// Logisim project 6502.circ as structural Verilog: 8 circuits, main circuit 6502
module _6502 (
  input  nNMI,
  input  nIRQ,
  input  RDY,
  input  nRES,
  input  SO,
  output PHI1,
  output PHI2,
  output R_W,
  output SYNC
);

  wire d_ff_1_qn, DECODER__0, DECODER__1, DECODER__2, DECODER__3, DECODER__4, DECODER__5, DECODER__6,
       DECODER__7, DECODER__8, DECODER__9, DECODER__10, DECODER__11, DECODER__12, DECODER__13, DECODER__14,
       DECODER__15, DECODER__16, DECODER__17, DECODER__18, DECODER__19, DECODER__20, DECODER__21,
       DECODER__23, DECODER__24, DECODER__25, DECODER__26, DECODER__27, DECODER__28, DECODER__29,
       DECODER__30, DECODER__31, DECODER__32, DECODER__33, DECODER__34, DECODER__35, DECODER__36,
       DECODER__37, DECODER__38, DECODER__39, DECODER__40, DECODER__41, DECODER__42, DECODER__43,
       DECODER__44, DECODER__45, DECODER__46, DECODER__47, DECODER__48, DECODER__49, DECODER__50,
       DECODER__51, DECODER__52, DECODER__53, DECODER__54, DECODER__55, DECODER__56, DECODER__57,
       DECODER__58, DECODER__59, DECODER__60, DECODER__61, DECODER__62, DECODER__63, DECODER__64,
       DECODER__65, DECODER__66, DECODER__67, DECODER__68, DECODER__69, DECODER__70, DECODER__71,
       DECODER__72, DECODER__73, DECODER__74, DECODER__75, DECODER__76, DECODER__77, DECODER__78,
       DECODER__79, DECODER__80, DECODER__81, DECODER__82, DECODER__83, DECODER__84, DECODER__85,
       DECODER__86, DECODER__87, DECODER__88, DECODER__89, DECODER__90, DECODER__91, DECODER__92,
       DECODER__93, DECODER__94, DECODER__95, DECODER__96, DECODER__97, DECODER__98, DECODER__99,
       DECODER__100, DECODER__101, DECODER__102, DECODER__103, DECODER__104, DECODER__105, DECODER__106,
       DECODER__107, DECODER__108, DECODER__109, DECODER__110, DECODER__111, DECODER__112, DECODER__113,
       DECODER__114, DECODER__115, DECODER__116, DECODER__117, DECODER__118, DECODER__119, DECODER__120,
       DECODER__121, DECODER__122, DECODER__123, DECODER__124, DECODER__125, DECODER__126, DECODER__127,
       DECODER__128, DECODER__129, IR_ir0, IR_ir1, IR_ir2, IR_ir3, IR_ir4, IR_ir5, IR_ir6, IR_ir7, PHI0_out,
       PREDECODE_implied, PREDECODE_pd0, PREDECODE_pd1, PREDECODE_pd2, PREDECODE_pd3, PREDECODE_pd4,
       PREDECODE_pd5, PREDECODE_pd6, PREDECODE_pd7, PREDECODE_twocycle, RANDOM_LOGIC__0_ir,
       RANDOM_LOGIC_fetch, RANDOM_LOGIC_t0, RANDOM_LOGIC_t1, RANDOM_LOGIC_t2, RANDOM_LOGIC_t3,
       RANDOM_LOGIC_t4, RANDOM_LOGIC_t5, RANDOM_LOGIC_wr;

  buf buffer_1 (SYNC, RANDOM_LOGIC_t1);
  D_Flip_Flop #(.trigger("high")) d_ff_1 (.clk(PHI2), .D(nNMI), .Qn(d_ff_1_qn));  // open: Q, preset, en, reset
  DECODER_TRANS DECODER (
    .T5(RANDOM_LOGIC_t5), .T4(RANDOM_LOGIC_t4), .T3(RANDOM_LOGIC_t3), .T2(RANDOM_LOGIC_t2), .IR0(IR_ir0),
    .IR1(IR_ir1), .IR7(IR_ir7), .IR4(IR_ir4), .IR3(IR_ir3), .IR2(IR_ir2), .IR6(IR_ir6), .IR5(IR_ir5),
    .T0(RANDOM_LOGIC_t0), .T1(RANDOM_LOGIC_t1), ._0(DECODER__0), ._1(DECODER__1), ._2(DECODER__2),
    ._3(DECODER__3), ._4(DECODER__4), ._5(DECODER__5), ._6(DECODER__6), ._7(DECODER__7), ._8(DECODER__8),
    ._9(DECODER__9), ._10(DECODER__10), ._11(DECODER__11), ._12(DECODER__12), ._13(DECODER__13),
    ._14(DECODER__14), ._15(DECODER__15), ._16(DECODER__16), ._17(DECODER__17), ._18(DECODER__18),
    ._19(DECODER__19), ._20(DECODER__20), ._21(DECODER__21), ._22(DECODER__21), ._23(DECODER__23),
    ._24(DECODER__24), ._25(DECODER__25), ._26(DECODER__26), ._27(DECODER__27), ._28(DECODER__28),
    ._29(DECODER__29), ._30(DECODER__30), ._31(DECODER__31), ._32(DECODER__32), ._33(DECODER__33),
    ._34(DECODER__34), ._35(DECODER__35), ._36(DECODER__36), ._37(DECODER__37), ._38(DECODER__38),
    ._39(DECODER__39), ._40(DECODER__40), ._41(DECODER__41), ._42(DECODER__42), ._43(DECODER__43),
    ._44(DECODER__44), ._45(DECODER__45), ._46(DECODER__46), ._47(DECODER__47), ._48(DECODER__48),
    ._49(DECODER__49), ._50(DECODER__50), ._51(DECODER__51), ._52(DECODER__52), ._53(DECODER__53),
    ._54(DECODER__54), ._55(DECODER__55), ._56(DECODER__56), ._57(DECODER__57), ._58(DECODER__58),
    ._59(DECODER__59), ._60(DECODER__60), ._61(DECODER__61), ._62(DECODER__62), ._63(DECODER__63),
    ._64(DECODER__64), ._65(DECODER__65), ._66(DECODER__66), ._67(DECODER__67), ._68(DECODER__68),
    ._69(DECODER__69), ._70(DECODER__70), ._71(DECODER__71), ._72(DECODER__72), ._73(DECODER__73),
    ._74(DECODER__74), ._75(DECODER__75), ._76(DECODER__76), ._77(DECODER__77), ._78(DECODER__78),
    ._79(DECODER__79), ._80(DECODER__80), ._81(DECODER__81), ._82(DECODER__82), ._83(DECODER__83),
    ._84(DECODER__84), ._85(DECODER__85), ._86(DECODER__86), ._87(DECODER__87), ._88(DECODER__88),
    ._89(DECODER__89), ._90(DECODER__90), ._91(DECODER__91), ._92(DECODER__92), ._93(DECODER__93),
    ._94(DECODER__94), ._95(DECODER__95), ._96(DECODER__96), ._97(DECODER__97), ._98(DECODER__98),
    ._99(DECODER__99), ._100(DECODER__100), ._101(DECODER__101), ._102(DECODER__102), ._103(DECODER__103),
    ._104(DECODER__104), ._105(DECODER__105), ._106(DECODER__106), ._107(DECODER__107), ._108(DECODER__108),
    ._109(DECODER__109), ._110(DECODER__110), ._111(DECODER__111), ._112(DECODER__112), ._113(DECODER__113),
    ._114(DECODER__114), ._115(DECODER__115), ._116(DECODER__116), ._117(DECODER__117), ._118(DECODER__118),
    ._119(DECODER__119), ._120(DECODER__120), ._121(DECODER__121), ._122(DECODER__122), ._123(DECODER__123),
    ._124(DECODER__124), ._125(DECODER__125), ._126(DECODER__126), ._127(DECODER__127), ._128(DECODER__128),
    ._129(DECODER__129));
  RANDOM_LOGIC RANDOM_LOGIC (
    .X0(DECODER__0), .X1(DECODER__1), .X2(DECODER__2), .X3(DECODER__3), .X4(DECODER__4), .X5(DECODER__5),
    .X6(DECODER__6), .X7(DECODER__7), .X8(DECODER__8), .X9(DECODER__9), .X10(DECODER__10), .X11(DECODER__11),
    .X12(DECODER__12), .X13(DECODER__13), .X14(DECODER__14), .X15(DECODER__15), .X16(DECODER__16),
    .X17(DECODER__17), .X18(DECODER__18), .X19(DECODER__19), .X20(DECODER__20), .X21(DECODER__21),
    .X22(DECODER__21), .X23(DECODER__23), .X24(DECODER__24), .X25(DECODER__25), .X26(DECODER__26),
    .X27(DECODER__27), .X28(DECODER__28), .X29(DECODER__29), .X30(DECODER__30), .X31(DECODER__31),
    .X32(DECODER__32), .X33(DECODER__33), .X34(DECODER__34), .X35(DECODER__35), .X36(DECODER__36),
    .X37(DECODER__37), .X38(DECODER__38), .X39(DECODER__39), .X40(DECODER__40), .X41(DECODER__41),
    .X42(DECODER__42), .X43(DECODER__43), .X44(DECODER__44), .X45(DECODER__45), .X46(DECODER__46),
    .X47(DECODER__47), .X48(DECODER__48), .X49(DECODER__49), .X50(DECODER__50), .X51(DECODER__51),
    .X52(DECODER__52), .X53(DECODER__53), .X54(DECODER__54), .X55(DECODER__55), .X56(DECODER__56),
    .X57(DECODER__57), .X58(DECODER__58), .X59(DECODER__59), .X60(DECODER__60), .X61(DECODER__61),
    .X62(DECODER__62), .X63(DECODER__63), .X64(DECODER__64), .X65(DECODER__65), .X66(DECODER__66),
    .X67(DECODER__67), .X68(DECODER__68), .X69(DECODER__69), .X70(DECODER__70), .X71(DECODER__71),
    .X72(DECODER__72), .X73(DECODER__73), .X74(DECODER__74), .X75(DECODER__75), .X76(DECODER__76),
    .X77(DECODER__77), .X78(DECODER__78), .X79(DECODER__79), .X80(DECODER__80), .X81(DECODER__81),
    .X82(DECODER__82), .X83(DECODER__83), .X84(DECODER__84), .X85(DECODER__85), .X86(DECODER__86),
    .X87(DECODER__87), .X88(DECODER__88), .X89(DECODER__89), .X90(DECODER__90), .X91(DECODER__91),
    .X92(DECODER__92), .X93(DECODER__93), .X94(DECODER__94), .X95(DECODER__95), .X96(DECODER__96),
    .X97(DECODER__97), .X98(DECODER__98), .X99(DECODER__99), .X100(DECODER__100), .X101(DECODER__101),
    .X102(DECODER__102), .X103(DECODER__103), .X104(DECODER__104), .X105(DECODER__105), .X106(DECODER__106),
    .X107(DECODER__107), .X108(DECODER__108), .X109(DECODER__109), .X110(DECODER__110), .X111(DECODER__111),
    .X112(DECODER__112), .X113(DECODER__113), .X114(DECODER__114), .X115(DECODER__115), .X116(DECODER__116),
    .X117(DECODER__117), .X118(DECODER__118), .X119(DECODER__119), .X120(DECODER__120), .X121(DECODER__121),
    .X122(DECODER__122), .X123(DECODER__123), .X124(DECODER__124), .X125(DECODER__125), .X126(DECODER__126),
    .X127(DECODER__127), .X128(DECODER__128), .X129(DECODER__129), .NMIP(d_ff_1_qn), .T0(RANDOM_LOGIC_t0),
    .T1(RANDOM_LOGIC_t1), .T2(RANDOM_LOGIC_t2), .T3(RANDOM_LOGIC_t3), .T4(RANDOM_LOGIC_t4),
    .T5(RANDOM_LOGIC_t5), .PHI1(PHI1), .PHI2(PHI2), .TWOCYCLE(PREDECODE_twocycle),
    .IMPLIED(PREDECODE_implied), .FETCH(RANDOM_LOGIC_fetch), .WR(RANDOM_LOGIC_wr), ._0_IR(RANDOM_LOGIC__0_ir));  // open: IRQP, RESP, RDY, SO, DB0, DB1, DB2, DB3, DB4, DB5, DB6, DB7, AVR, ACR, ADH_ABH, ADL_ABL, Y_SB, X_SB, _0_ADL0, _0_ADL1, _0_ADL2, SB_Y, SB_X, S_SB, S_ADL, SB_S, S_S
  Clock PHI0 (.out(PHI0_out));
  CLOCKGEN clockgen_1 (.PHI0(PHI0_out), .PHI2(PHI2), .PHI1(PHI1));
  D_latch RWLatch (.EN(PHI1), .D(RANDOM_LOGIC_wr), .NOT_Q(R_W));  // open: Q
  IR IR (
    .FETCH(RANDOM_LOGIC_fetch), .PHI1(PHI1), .in0(PREDECODE_pd0), .in1(PREDECODE_pd1), .in2(PREDECODE_pd2),
    .in3(PREDECODE_pd3), .in4(PREDECODE_pd4), .in5(PREDECODE_pd5), .in6(PREDECODE_pd6), .in7(PREDECODE_pd7),
    .IR0(IR_ir0), .IR2(IR_ir2), .IR3(IR_ir3), .IR4(IR_ir4), .IR5(IR_ir5), .IR6(IR_ir6), .IR7(IR_ir7),
    .IR1(IR_ir1));
  PREDECODE PREDECODE (
    .PHI2(PHI2), ._0_IR(RANDOM_LOGIC__0_ir), .PD0(PREDECODE_pd0), .PD1(PREDECODE_pd1), .PD2(PREDECODE_pd2),
    .PD3(PREDECODE_pd3), .PD4(PREDECODE_pd4), .PD5(PREDECODE_pd5), .PD6(PREDECODE_pd6), .PD7(PREDECODE_pd7),
    .IMPLIED(PREDECODE_implied), .TWOCYCLE(PREDECODE_twocycle));  // open: D0, D1, D2, D3, D4, D5, D6, D7

  // Notes on the sheet:
  //   PHI2
  //   PHI1
  //   NMIP
  //   PHI2
  //   PHI1
  //   PHI1
  //   PHI2
endmodule

module CLOCKGEN (
  input  PHI0,
  output PHI2,
  output PHI1
);

  wire not_1_out;

  not not_1 (not_1_out, PHI0);
  not not_2 (PHI1, PHI0);
  not not_3 (PHI2, not_1_out);
endmodule

module IR (
  input  FETCH,
  input  PHI1,
  input  in0,
  input  in1,
  input  in2,
  input  in3,
  input  in4,
  input  in5,
  input  in6,
  input  in7,
  output IR0,
  output IR1,
  output IR2,
  output IR3,
  output IR4,
  output IR5,
  output IR6,
  output IR7
);

  wire and_1_out;

  and and_1 (and_1_out, FETCH, PHI1);
  D_latch d_latch_1 (.EN(and_1_out), .D(in0), .Q(IR0));  // open: NOT_Q
  D_latch d_latch_2 (.EN(and_1_out), .D(in1), .Q(IR1));  // open: NOT_Q
  D_latch d_latch_3 (.EN(and_1_out), .D(in2), .Q(IR2));  // open: NOT_Q
  D_latch d_latch_4 (.EN(and_1_out), .D(in3), .Q(IR3));  // open: NOT_Q
  D_latch d_latch_5 (.EN(and_1_out), .D(in4), .Q(IR4));  // open: NOT_Q
  D_latch d_latch_6 (.EN(and_1_out), .D(in5), .Q(IR5));  // open: NOT_Q
  D_latch d_latch_7 (.EN(and_1_out), .D(in6), .Q(IR6));  // open: NOT_Q
  D_latch d_latch_8 (.EN(and_1_out), .D(in7), .Q(IR7));  // open: NOT_Q
endmodule

module DECODER_TRANS (
  input  T5,
  input  T4,
  input  T3,
  input  T2,
  input  IR0,
  input  IR1,
  input  IR7,
  input  IR4,
  input  IR3,
  input  IR2,
  input  IR6,
  input  IR5,
  input  T0,
  input  T1,
  output _0,
  output _1,
  output _2,
  output _3,
  output _4,
  output _5,
  output _6,
  output _7,
  output _8,
  output _9,
  output _10,
  output _11,
  output _12,
  output _13,
  output _14,
  output _15,
  output _16,
  output _17,
  output _18,
  output _19,
  output _20,
  output _21,
  output _22,
  output _23,
  output _24,
  output _25,
  output _26,
  output _27,
  output _28,
  output _29,
  output _30,
  output _31,
  output _32,
  output _33,
  output _34,
  output _35,
  output _36,
  output _37,
  output _38,
  output _39,
  output _40,
  output _41,
  output _42,
  output _43,
  output _44,
  output _45,
  output _46,
  output _47,
  output _48,
  output _49,
  output _50,
  output _51,
  output _52,
  output _53,
  output _54,
  output _55,
  output _56,
  output _57,
  output _58,
  output _59,
  output _60,
  output _61,
  output _62,
  output _63,
  output _64,
  output _65,
  output _66,
  output _67,
  output _68,
  output _69,
  output _70,
  output _71,
  output _72,
  output _73,
  output _74,
  output _75,
  output _76,
  output _77,
  output _78,
  output _79,
  output _80,
  output _81,
  output _82,
  output _83,
  output _84,
  output _85,
  output _86,
  output _87,
  output _88,
  output _89,
  output _90,
  output _91,
  output _92,
  output _93,
  output _94,
  output _95,
  output _96,
  output _97,
  output _98,
  output _99,
  output _100,
  output _101,
  output _102,
  output _103,
  output _104,
  output _105,
  output _106,
  output _107,
  output _108,
  output _109,
  output _110,
  output _111,
  output _112,
  output _113,
  output _114,
  output _115,
  output _116,
  output _117,
  output _118,
  output _119,
  output _120,
  output _121,
  output _122,
  output _123,
  output _124,
  output _125,
  output _126,
  output _127,
  output _128,
  output _129
);

  wire not_1_out, not_2_out, not_3_out, not_4_out, not_5_out, not_6_out, not_7_out, not_8_out, not_9_out,
       not_10_out, not_11_out, not_12_out, not_13_out, not_14_out, or_1_out;

  not not_1 (not_1_out, T5);
  not not_2 (not_2_out, T4);
  not not_3 (not_3_out, T3);
  not not_4 (not_4_out, T2);
  not not_5 (not_5_out, IR1);
  or or_1 (or_1_out, IR0, IR1);
  not not_6 (not_6_out, IR0);
  not not_7 (not_7_out, IR7);
  not not_8 (not_8_out, IR4);
  not not_9 (not_9_out, IR3);
  not not_10 (not_10_out, IR2);
  not not_11 (not_11_out, IR6);
  not not_12 (not_12_out, IR5);
  not not_13 (not_13_out, T0);
  not not_14 (not_14_out, T1);
  Pull_Resistor #(.pull(1)) pull_resistor_1 (.node(_0));
  Pull_Resistor #(.pull(1)) pull_resistor_2 (.node(_1));
  Transistor #(.\type ("n")) transistor_1 (.in(1'b0), .out(_1), .gate(not_3_out));
  Transistor #(.\type ("n")) transistor_2 (.in(1'b0), .out(_0), .gate(or_1_out));
  Transistor #(.\type ("n")) transistor_3 (.in(1'b0), .out(_1), .gate(not_6_out));
  Transistor #(.\type ("n")) transistor_4 (.in(1'b0), .out(_0), .gate(not_7_out));
  Transistor #(.\type ("n")) transistor_5 (.in(1'b0), .out(_1), .gate(not_8_out));
  Transistor #(.\type ("n")) transistor_6 (.in(1'b0), .out(_0), .gate(not_8_out));
  Transistor #(.\type ("n")) transistor_7 (.in(1'b0), .out(_1), .gate(IR3));
  Transistor #(.\type ("n")) transistor_8 (.in(1'b0), .out(_1), .gate(IR2));
  Transistor #(.\type ("n")) transistor_9 (.in(1'b0), .out(_0), .gate(not_10_out));
  Transistor #(.\type ("n")) transistor_10 (.in(1'b0), .out(_0), .gate(IR6));
  Transistor #(.\type ("n")) transistor_11 (.in(1'b0), .out(_0), .gate(IR5));
  Pull_Resistor #(.pull(1)) pull_resistor_3 (.node(_2));
  Transistor #(.\type ("n")) transistor_12 (.in(1'b0), .out(_2), .gate(not_4_out));
  Transistor #(.\type ("n")) transistor_13 (.in(1'b0), .out(_2), .gate(not_6_out));
  Transistor #(.\type ("n")) transistor_14 (.in(1'b0), .out(_2), .gate(not_8_out));
  Transistor #(.\type ("n")) transistor_15 (.in(1'b0), .out(_2), .gate(not_9_out));
  Transistor #(.\type ("n")) transistor_16 (.in(1'b0), .out(_2), .gate(IR2));
  Pull_Resistor #(.pull(1)) pull_resistor_4 (.node(_3));
  Transistor #(.\type ("n")) transistor_17 (.in(1'b0), .out(_3), .gate(or_1_out));
  Transistor #(.\type ("n")) transistor_18 (.in(1'b0), .out(_3), .gate(not_7_out));
  Transistor #(.\type ("n")) transistor_19 (.in(1'b0), .out(_3), .gate(IR4));
  Transistor #(.\type ("n")) transistor_20 (.in(1'b0), .out(_3), .gate(not_9_out));
  Transistor #(.\type ("n")) transistor_21 (.in(1'b0), .out(_3), .gate(IR2));
  Transistor #(.\type ("n")) transistor_22 (.in(1'b0), .out(_3), .gate(IR5));
  Transistor #(.\type ("n")) transistor_23 (.in(1'b0), .out(_3), .gate(not_13_out));
  Pull_Resistor #(.pull(1)) pull_resistor_5 (.node(_4));
  Pull_Resistor #(.pull(1)) pull_resistor_6 (.node(_5));
  Transistor #(.\type ("n")) transistor_24 (.in(1'b0), .out(_5), .gate(or_1_out));
  Transistor #(.\type ("n")) transistor_25 (.in(1'b0), .out(_4), .gate(or_1_out));
  Transistor #(.\type ("n")) transistor_26 (.in(1'b0), .out(_4), .gate(not_7_out));
  Transistor #(.\type ("n")) transistor_27 (.in(1'b0), .out(_5), .gate(not_7_out));
  Transistor #(.\type ("n")) transistor_28 (.in(1'b0), .out(_5), .gate(IR4));
  Transistor #(.\type ("n")) transistor_29 (.in(1'b0), .out(_4), .gate(not_8_out));
  Transistor #(.\type ("n")) transistor_30 (.in(1'b0), .out(_4), .gate(not_9_out));
  Transistor #(.\type ("n")) transistor_31 (.in(1'b0), .out(_4), .gate(IR2));
  Transistor #(.\type ("n")) transistor_32 (.in(1'b0), .out(_4), .gate(IR6));
  Transistor #(.\type ("n")) transistor_33 (.in(1'b0), .out(_5), .gate(not_11_out));
  Transistor #(.\type ("n")) transistor_34 (.in(1'b0), .out(_5), .gate(IR5));
  Transistor #(.\type ("n")) transistor_35 (.in(1'b0), .out(_4), .gate(IR5));
  Transistor #(.\type ("n")) transistor_36 (.in(1'b0), .out(_5), .gate(not_13_out));
  Transistor #(.\type ("n")) transistor_37 (.in(1'b0), .out(_4), .gate(not_13_out));
  Pull_Resistor #(.pull(1)) pull_resistor_7 (.node(_6));
  Transistor #(.\type ("n")) transistor_38 (.in(1'b0), .out(_6), .gate(not_4_out));
  Transistor #(.\type ("n")) transistor_39 (.in(1'b0), .out(_6), .gate(not_8_out));
  Transistor #(.\type ("n")) transistor_40 (.in(1'b0), .out(_6), .gate(not_10_out));
  Pull_Resistor #(.pull(1)) pull_resistor_8 (.node(_7));
  Transistor #(.\type ("n")) transistor_41 (.in(1'b0), .out(_7), .gate(not_5_out));
  Transistor #(.\type ("n")) transistor_42 (.in(1'b0), .out(_7), .gate(not_7_out));
  Transistor #(.\type ("n")) transistor_43 (.in(1'b0), .out(_7), .gate(IR6));
  Pull_Resistor #(.pull(1)) pull_resistor_9 (.node(_8));
  Pull_Resistor #(.pull(1)) pull_resistor_10 (.node(_9));
  Transistor #(.\type ("n")) transistor_44 (.in(1'b0), .out(_8), .gate(not_4_out));
  Transistor #(.\type ("n")) transistor_45 (.in(1'b0), .out(_9), .gate(not_5_out));
  Transistor #(.\type ("n")) transistor_46 (.in(1'b0), .out(_8), .gate(not_6_out));
  Transistor #(.\type ("n")) transistor_47 (.in(1'b0), .out(_9), .gate(not_7_out));
  Transistor #(.\type ("n")) transistor_48 (.in(1'b0), .out(_9), .gate(IR4));
  Transistor #(.\type ("n")) transistor_49 (.in(1'b0), .out(_8), .gate(IR4));
  Transistor #(.\type ("n")) transistor_50 (.in(1'b0), .out(_8), .gate(IR3));
  Transistor #(.\type ("n")) transistor_51 (.in(1'b0), .out(_9), .gate(not_9_out));
  Transistor #(.\type ("n")) transistor_52 (.in(1'b0), .out(_9), .gate(IR2));
  Transistor #(.\type ("n")) transistor_53 (.in(1'b0), .out(_8), .gate(IR2));
  Transistor #(.\type ("n")) transistor_54 (.in(1'b0), .out(_9), .gate(IR6));
  Transistor #(.\type ("n")) transistor_55 (.in(1'b0), .out(_9), .gate(IR5));
  Transistor #(.\type ("n")) transistor_56 (.in(1'b0), .out(_9), .gate(not_13_out));
  Pull_Resistor #(.pull(1)) pull_resistor_11 (.node(_10));
  Transistor #(.\type ("n")) transistor_57 (.in(1'b0), .out(_10), .gate(not_5_out));
  Transistor #(.\type ("n")) transistor_58 (.in(1'b0), .out(_10), .gate(not_7_out));
  Transistor #(.\type ("n")) transistor_59 (.in(1'b0), .out(_10), .gate(IR4));
  Transistor #(.\type ("n")) transistor_60 (.in(1'b0), .out(_10), .gate(not_9_out));
  Transistor #(.\type ("n")) transistor_61 (.in(1'b0), .out(_10), .gate(IR2));
  Transistor #(.\type ("n")) transistor_62 (.in(1'b0), .out(_10), .gate(not_11_out));
  Transistor #(.\type ("n")) transistor_63 (.in(1'b0), .out(_10), .gate(IR5));
  Transistor #(.\type ("n")) transistor_64 (.in(1'b0), .out(_10), .gate(not_13_out));
  Pull_Resistor #(.pull(1)) pull_resistor_12 (.node(_11));
  Transistor #(.\type ("n")) transistor_65 (.in(1'b0), .out(_11), .gate(or_1_out));
  Transistor #(.\type ("n")) transistor_66 (.in(1'b0), .out(_11), .gate(not_7_out));
  Transistor #(.\type ("n")) transistor_67 (.in(1'b0), .out(_11), .gate(IR4));
  Transistor #(.\type ("n")) transistor_68 (.in(1'b0), .out(_11), .gate(not_11_out));
  Transistor #(.\type ("n")) transistor_69 (.in(1'b0), .out(_11), .gate(not_12_out));
  Transistor #(.\type ("n")) transistor_70 (.in(1'b0), .out(_11), .gate(not_13_out));
  Pull_Resistor #(.pull(1)) pull_resistor_13 (.node(_12));
  Pull_Resistor #(.pull(1)) pull_resistor_14 (.node(_13));
  Transistor #(.\type ("n")) transistor_71 (.in(1'b0), .out(_13), .gate(not_5_out));
  Transistor #(.\type ("n")) transistor_72 (.in(1'b0), .out(_12), .gate(not_5_out));
  Transistor #(.\type ("n")) transistor_73 (.in(1'b0), .out(_12), .gate(not_7_out));
  Transistor #(.\type ("n")) transistor_74 (.in(1'b0), .out(_13), .gate(not_7_out));
  Transistor #(.\type ("n")) transistor_75 (.in(1'b0), .out(_13), .gate(not_8_out));
  Transistor #(.\type ("n")) transistor_76 (.in(1'b0), .out(_13), .gate(not_9_out));
  Transistor #(.\type ("n")) transistor_77 (.in(1'b0), .out(_13), .gate(IR2));
  Transistor #(.\type ("n")) transistor_78 (.in(1'b0), .out(_12), .gate(IR6));
  Transistor #(.\type ("n")) transistor_79 (.in(1'b0), .out(_13), .gate(IR6));
  Transistor #(.\type ("n")) transistor_80 (.in(1'b0), .out(_13), .gate(IR5));
  Transistor #(.\type ("n")) transistor_81 (.in(1'b0), .out(_12), .gate(IR5));
  Transistor #(.\type ("n")) transistor_82 (.in(1'b0), .out(_13), .gate(not_13_out));
  Pull_Resistor #(.pull(1)) pull_resistor_15 (.node(_14));
  Transistor #(.\type ("n")) transistor_83 (.in(1'b0), .out(_14), .gate(not_5_out));
  Transistor #(.\type ("n")) transistor_84 (.in(1'b0), .out(_14), .gate(not_7_out));
  Transistor #(.\type ("n")) transistor_85 (.in(1'b0), .out(_14), .gate(IR6));
  Transistor #(.\type ("n")) transistor_86 (.in(1'b0), .out(_14), .gate(not_12_out));
  Transistor #(.\type ("n")) transistor_87 (.in(1'b0), .out(_14), .gate(not_13_out));
  Pull_Resistor #(.pull(1)) pull_resistor_16 (.node(_15));
  Transistor #(.\type ("n")) transistor_88 (.in(1'b0), .out(_15), .gate(not_5_out));
  Transistor #(.\type ("n")) transistor_89 (.in(1'b0), .out(_15), .gate(not_7_out));
  Transistor #(.\type ("n")) transistor_90 (.in(1'b0), .out(_15), .gate(IR4));
  Transistor #(.\type ("n")) transistor_91 (.in(1'b0), .out(_15), .gate(not_9_out));
  Transistor #(.\type ("n")) transistor_92 (.in(1'b0), .out(_15), .gate(IR2));
  Transistor #(.\type ("n")) transistor_93 (.in(1'b0), .out(_15), .gate(not_11_out));
  Transistor #(.\type ("n")) transistor_94 (.in(1'b0), .out(_15), .gate(IR5));
  Transistor #(.\type ("n")) transistor_95 (.in(1'b0), .out(_15), .gate(not_14_out));
  Pull_Resistor #(.pull(1)) pull_resistor_17 (.node(_16));
  Pull_Resistor #(.pull(1)) pull_resistor_18 (.node(_17));
  Transistor #(.\type ("n")) transistor_96 (.in(1'b0), .out(_17), .gate(not_5_out));
  Transistor #(.\type ("n")) transistor_97 (.in(1'b0), .out(_16), .gate(or_1_out));
  Transistor #(.\type ("n")) transistor_98 (.in(1'b0), .out(_16), .gate(not_7_out));
  Transistor #(.\type ("n")) transistor_99 (.in(1'b0), .out(_17), .gate(not_7_out));
  Transistor #(.\type ("n")) transistor_100 (.in(1'b0), .out(_16), .gate(IR4));
  Transistor #(.\type ("n")) transistor_101 (.in(1'b0), .out(_17), .gate(not_8_out));
  Transistor #(.\type ("n")) transistor_102 (.in(1'b0), .out(_17), .gate(not_9_out));
  Transistor #(.\type ("n")) transistor_103 (.in(1'b0), .out(_16), .gate(not_9_out));
  Transistor #(.\type ("n")) transistor_104 (.in(1'b0), .out(_17), .gate(IR2));
  Transistor #(.\type ("n")) transistor_105 (.in(1'b0), .out(_16), .gate(IR2));
  Transistor #(.\type ("n")) transistor_106 (.in(1'b0), .out(_17), .gate(IR6));
  Transistor #(.\type ("n")) transistor_107 (.in(1'b0), .out(_16), .gate(not_11_out));
  Transistor #(.\type ("n")) transistor_108 (.in(1'b0), .out(_17), .gate(not_12_out));
  Transistor #(.\type ("n")) transistor_109 (.in(1'b0), .out(_16), .gate(not_12_out));
  Transistor #(.\type ("n")) transistor_110 (.in(1'b0), .out(_17), .gate(not_13_out));
  Transistor #(.\type ("n")) transistor_111 (.in(1'b0), .out(_16), .gate(not_14_out));
  Pull_Resistor #(.pull(1)) pull_resistor_19 (.node(_18));
  Transistor #(.\type ("n")) transistor_112 (.in(1'b0), .out(_18), .gate(or_1_out));
  Transistor #(.\type ("n")) transistor_113 (.in(1'b0), .out(_18), .gate(not_7_out));
  Transistor #(.\type ("n")) transistor_114 (.in(1'b0), .out(_18), .gate(IR4));
  Transistor #(.\type ("n")) transistor_115 (.in(1'b0), .out(_18), .gate(not_9_out));
  Transistor #(.\type ("n")) transistor_116 (.in(1'b0), .out(_18), .gate(IR2));
  Transistor #(.\type ("n")) transistor_117 (.in(1'b0), .out(_18), .gate(IR5));
  Transistor #(.\type ("n")) transistor_118 (.in(1'b0), .out(_18), .gate(not_14_out));
  Pull_Resistor #(.pull(1)) pull_resistor_20 (.node(_19));
  Transistor #(.\type ("n")) transistor_119 (.in(1'b0), .out(_19), .gate(or_1_out));
  Transistor #(.\type ("n")) transistor_120 (.in(1'b0), .out(_19), .gate(not_7_out));
  Transistor #(.\type ("n")) transistor_121 (.in(1'b0), .out(_19), .gate(not_10_out));
  Transistor #(.\type ("n")) transistor_122 (.in(1'b0), .out(_19), .gate(IR6));
  Transistor #(.\type ("n")) transistor_123 (.in(1'b0), .out(_19), .gate(not_12_out));
  Transistor #(.\type ("n")) transistor_124 (.in(1'b0), .out(_19), .gate(not_13_out));
  Pull_Resistor #(.pull(1)) pull_resistor_21 (.node(_20));
  Transistor #(.\type ("n")) transistor_125 (.in(1'b0), .out(_20), .gate(or_1_out));
  Transistor #(.\type ("n")) transistor_126 (.in(1'b0), .out(_20), .gate(not_7_out));
  Transistor #(.\type ("n")) transistor_127 (.in(1'b0), .out(_20), .gate(IR4));
  Transistor #(.\type ("n")) transistor_128 (.in(1'b0), .out(_20), .gate(IR6));
  Transistor #(.\type ("n")) transistor_129 (.in(1'b0), .out(_20), .gate(not_12_out));
  Transistor #(.\type ("n")) transistor_130 (.in(1'b0), .out(_20), .gate(not_13_out));
  Pull_Resistor #(.pull(1)) pull_resistor_22 (.node(_21));
  Transistor #(.\type ("n")) transistor_131 (.in(1'b0), .out(_21), .gate(or_1_out));
  Transistor #(.\type ("n")) transistor_132 (.in(1'b0), .out(_21), .gate(IR7));
  Transistor #(.\type ("n")) transistor_133 (.in(1'b0), .out(_21), .gate(IR4));
  Transistor #(.\type ("n")) transistor_134 (.in(1'b0), .out(_21), .gate(IR3));
  Transistor #(.\type ("n")) transistor_135 (.in(1'b0), .out(_21), .gate(IR2));
  Transistor #(.\type ("n")) transistor_136 (.in(1'b0), .out(_21), .gate(IR6));
  Transistor #(.\type ("n")) transistor_137 (.in(1'b0), .out(_21), .gate(not_12_out));
  Transistor #(.\type ("n")) transistor_138 (.in(1'b0), .out(_21), .gate(not_13_out));
  Pull_Resistor #(.pull(1)) pull_resistor_23 (.node(_22));
  Transistor #(.\type ("n")) transistor_139 (.in(1'b0), .out(_22), .gate(not_1_out));
  Transistor #(.\type ("n")) transistor_140 (.in(1'b0), .out(_22), .gate(or_1_out));
  Transistor #(.\type ("n")) transistor_141 (.in(1'b0), .out(_22), .gate(IR7));
  Transistor #(.\type ("n")) transistor_142 (.in(1'b0), .out(_22), .gate(IR4));
  Transistor #(.\type ("n")) transistor_143 (.in(1'b0), .out(_22), .gate(IR3));
  Transistor #(.\type ("n")) transistor_144 (.in(1'b0), .out(_22), .gate(IR2));
  Transistor #(.\type ("n")) transistor_145 (.in(1'b0), .out(_22), .gate(IR6));
  Transistor #(.\type ("n")) transistor_146 (.in(1'b0), .out(_22), .gate(IR5));
  Pull_Resistor #(.pull(1)) pull_resistor_24 (.node(_23));
  Transistor #(.\type ("n")) transistor_147 (.in(1'b0), .out(_23), .gate(or_1_out));
  Transistor #(.\type ("n")) transistor_148 (.in(1'b0), .out(_23), .gate(IR7));
  Transistor #(.\type ("n")) transistor_149 (.in(1'b0), .out(_23), .gate(IR4));
  Transistor #(.\type ("n")) transistor_150 (.in(1'b0), .out(_23), .gate(not_9_out));
  Transistor #(.\type ("n")) transistor_151 (.in(1'b0), .out(_23), .gate(IR2));
  Transistor #(.\type ("n")) transistor_152 (.in(1'b0), .out(_23), .gate(IR5));
  Transistor #(.\type ("n")) transistor_153 (.in(1'b0), .out(_23), .gate(not_13_out));
  Pull_Resistor #(.pull(1)) pull_resistor_25 (.node(_25));
  Pull_Resistor #(.pull(1)) pull_resistor_26 (.node(_24));
  Transistor #(.\type ("n")) transistor_154 (.in(1'b0), .out(_24), .gate(not_2_out));
  Transistor #(.\type ("n")) transistor_155 (.in(1'b0), .out(_25), .gate(not_3_out));
  Transistor #(.\type ("n")) transistor_156 (.in(1'b0), .out(_24), .gate(or_1_out));
  Transistor #(.\type ("n")) transistor_157 (.in(1'b0), .out(_25), .gate(or_1_out));
  Transistor #(.\type ("n")) transistor_158 (.in(1'b0), .out(_25), .gate(IR7));
  Transistor #(.\type ("n")) transistor_159 (.in(1'b0), .out(_24), .gate(IR7));
  Transistor #(.\type ("n")) transistor_160 (.in(1'b0), .out(_24), .gate(IR4));
  Transistor #(.\type ("n")) transistor_161 (.in(1'b0), .out(_25), .gate(IR4));
  Transistor #(.\type ("n")) transistor_162 (.in(1'b0), .out(_24), .gate(IR3));
  Transistor #(.\type ("n")) transistor_163 (.in(1'b0), .out(_25), .gate(not_9_out));
  Transistor #(.\type ("n")) transistor_164 (.in(1'b0), .out(_24), .gate(IR2));
  Transistor #(.\type ("n")) transistor_165 (.in(1'b0), .out(_25), .gate(IR2));
  Transistor #(.\type ("n")) transistor_166 (.in(1'b0), .out(_24), .gate(not_11_out));
  Transistor #(.\type ("n")) transistor_167 (.in(1'b0), .out(_24), .gate(not_12_out));
  Transistor #(.\type ("n")) transistor_168 (.in(1'b0), .out(_25), .gate(not_12_out));
  Pull_Resistor #(.pull(1)) pull_resistor_27 (.node(_26));
  Transistor #(.\type ("n")) transistor_169 (.in(1'b0), .out(_26), .gate(not_1_out));
  Transistor #(.\type ("n")) transistor_170 (.in(1'b0), .out(_26), .gate(or_1_out));
  Transistor #(.\type ("n")) transistor_171 (.in(1'b0), .out(_26), .gate(IR7));
  Transistor #(.\type ("n")) transistor_172 (.in(1'b0), .out(_26), .gate(IR4));
  Transistor #(.\type ("n")) transistor_173 (.in(1'b0), .out(_26), .gate(IR3));
  Transistor #(.\type ("n")) transistor_174 (.in(1'b0), .out(_26), .gate(IR2));
  Transistor #(.\type ("n")) transistor_175 (.in(1'b0), .out(_26), .gate(not_11_out));
  Transistor #(.\type ("n")) transistor_176 (.in(1'b0), .out(_26), .gate(IR5));
  Pull_Resistor #(.pull(1)) pull_resistor_28 (.node(_27));
  Transistor #(.\type ("n")) transistor_177 (.in(1'b0), .out(_27), .gate(not_5_out));
  Transistor #(.\type ("n")) transistor_178 (.in(1'b0), .out(_27), .gate(IR7));
  Transistor #(.\type ("n")) transistor_179 (.in(1'b0), .out(_27), .gate(not_11_out));
  Transistor #(.\type ("n")) transistor_180 (.in(1'b0), .out(_27), .gate(not_12_out));
  Pull_Resistor #(.pull(1)) pull_resistor_29 (.node(_28));
  Pull_Resistor #(.pull(1)) pull_resistor_30 (.node(_29));
  Transistor #(.\type ("n")) transistor_181 (.in(1'b0), .out(_28), .gate(not_4_out));
  Transistor #(.\type ("n")) transistor_182 (.in(1'b0), .out(_29), .gate(not_6_out));
  Transistor #(.\type ("n")) transistor_183 (.in(1'b0), .out(_29), .gate(IR7));
  Transistor #(.\type ("n")) transistor_184 (.in(1'b0), .out(_29), .gate(not_11_out));
  Transistor #(.\type ("n")) transistor_185 (.in(1'b0), .out(_29), .gate(IR5));
  Transistor #(.\type ("n")) transistor_186 (.in(1'b0), .out(_29), .gate(not_13_out));
  Pull_Resistor #(.pull(1)) pull_resistor_31 (.node(_30));
  Transistor #(.\type ("n")) transistor_187 (.in(1'b0), .out(_30), .gate(or_1_out));
  Transistor #(.\type ("n")) transistor_188 (.in(1'b0), .out(_30), .gate(IR7));
  Transistor #(.\type ("n")) transistor_189 (.in(1'b0), .out(_30), .gate(IR4));
  Transistor #(.\type ("n")) transistor_190 (.in(1'b0), .out(_30), .gate(not_9_out));
  Transistor #(.\type ("n")) transistor_191 (.in(1'b0), .out(_30), .gate(not_10_out));
  Transistor #(.\type ("n")) transistor_192 (.in(1'b0), .out(_30), .gate(not_11_out));
  Pull_Resistor #(.pull(1)) pull_resistor_32 (.node(_31));
  Transistor #(.\type ("n")) transistor_193 (.in(1'b0), .out(_31), .gate(not_4_out));
  Transistor #(.\type ("n")) transistor_194 (.in(1'b0), .out(_31), .gate(IR4));
  Transistor #(.\type ("n")) transistor_195 (.in(1'b0), .out(_31), .gate(not_9_out));
  Transistor #(.\type ("n")) transistor_196 (.in(1'b0), .out(_31), .gate(not_10_out));
  Pull_Resistor #(.pull(1)) pull_resistor_33 (.node(_32));
  Pull_Resistor #(.pull(1)) pull_resistor_34 (.node(_33));
  Transistor #(.\type ("n")) transistor_197 (.in(1'b0), .out(_33), .gate(not_4_out));
  Transistor #(.\type ("n")) transistor_198 (.in(1'b0), .out(_32), .gate(not_6_out));
  Transistor #(.\type ("n")) transistor_199 (.in(1'b0), .out(_32), .gate(IR7));
  Transistor #(.\type ("n")) transistor_200 (.in(1'b0), .out(_33), .gate(IR3));
  Transistor #(.\type ("n")) transistor_201 (.in(1'b0), .out(_32), .gate(IR6));
  Transistor #(.\type ("n")) transistor_202 (.in(1'b0), .out(_32), .gate(IR5));
  Transistor #(.\type ("n")) transistor_203 (.in(1'b0), .out(_32), .gate(not_13_out));
  Pull_Resistor #(.pull(1)) pull_resistor_35 (.node(_34));
  Transistor #(.\type ("n")) transistor_204 (.in(1'b0), .out(_34), .gate(not_13_out));
  Pull_Resistor #(.pull(1)) pull_resistor_36 (.node(_35));
  Transistor #(.\type ("n")) transistor_205 (.in(1'b0), .out(_35), .gate(not_4_out));
  Transistor #(.\type ("n")) transistor_206 (.in(1'b0), .out(_35), .gate(or_1_out));
  Transistor #(.\type ("n")) transistor_207 (.in(1'b0), .out(_35), .gate(IR7));
  Transistor #(.\type ("n")) transistor_208 (.in(1'b0), .out(_35), .gate(IR4));
  Transistor #(.\type ("n")) transistor_209 (.in(1'b0), .out(_35), .gate(IR2));
  Pull_Resistor #(.pull(1)) pull_resistor_37 (.node(_36));
  Transistor #(.\type ("n")) transistor_210 (.in(1'b0), .out(_36), .gate(not_3_out));
  Transistor #(.\type ("n")) transistor_211 (.in(1'b0), .out(_36), .gate(or_1_out));
  Transistor #(.\type ("n")) transistor_212 (.in(1'b0), .out(_36), .gate(IR7));
  Transistor #(.\type ("n")) transistor_213 (.in(1'b0), .out(_36), .gate(IR4));
  Pull_Resistor #(.pull(1)) pull_resistor_38 (.node(_37));
  Transistor #(.\type ("n")) transistor_214 (.in(1'b0), .out(_37), .gate(not_2_out));
  Transistor #(.\type ("n")) transistor_215 (.in(1'b0), .out(_37), .gate(or_1_out));
  Transistor #(.\type ("n")) transistor_216 (.in(1'b0), .out(_37), .gate(IR7));
  Transistor #(.\type ("n")) transistor_217 (.in(1'b0), .out(_37), .gate(IR4));
  Transistor #(.\type ("n")) transistor_218 (.in(1'b0), .out(_37), .gate(IR3));
  Transistor #(.\type ("n")) transistor_219 (.in(1'b0), .out(_37), .gate(IR2));
  Transistor #(.\type ("n")) transistor_220 (.in(1'b0), .out(_37), .gate(IR6));
  Pull_Resistor #(.pull(1)) pull_resistor_39 (.node(_38));
  Transistor #(.\type ("n")) transistor_221 (.in(1'b0), .out(_38), .gate(not_2_out));
  Transistor #(.\type ("n")) transistor_222 (.in(1'b0), .out(_38), .gate(or_1_out));
  Transistor #(.\type ("n")) transistor_223 (.in(1'b0), .out(_38), .gate(IR7));
  Transistor #(.\type ("n")) transistor_224 (.in(1'b0), .out(_38), .gate(IR4));
  Transistor #(.\type ("n")) transistor_225 (.in(1'b0), .out(_38), .gate(IR3));
  Transistor #(.\type ("n")) transistor_226 (.in(1'b0), .out(_38), .gate(IR2));
  Transistor #(.\type ("n")) transistor_227 (.in(1'b0), .out(_38), .gate(not_11_out));
  Transistor #(.\type ("n")) transistor_228 (.in(1'b0), .out(_38), .gate(IR5));
  Pull_Resistor #(.pull(1)) pull_resistor_40 (.node(_39));
  Pull_Resistor #(.pull(1)) pull_resistor_41 (.node(_40));
  Transistor #(.\type ("n")) transistor_229 (.in(1'b0), .out(_40), .gate(not_2_out));
  Transistor #(.\type ("n")) transistor_230 (.in(1'b0), .out(_39), .gate(not_3_out));
  Transistor #(.\type ("n")) transistor_231 (.in(1'b0), .out(_39), .gate(not_6_out));
  Transistor #(.\type ("n")) transistor_232 (.in(1'b0), .out(_40), .gate(not_6_out));
  Transistor #(.\type ("n")) transistor_233 (.in(1'b0), .out(_39), .gate(IR4));
  Transistor #(.\type ("n")) transistor_234 (.in(1'b0), .out(_40), .gate(not_8_out));
  Transistor #(.\type ("n")) transistor_235 (.in(1'b0), .out(_40), .gate(IR3));
  Transistor #(.\type ("n")) transistor_236 (.in(1'b0), .out(_39), .gate(IR3));
  Transistor #(.\type ("n")) transistor_237 (.in(1'b0), .out(_40), .gate(IR2));
  Transistor #(.\type ("n")) transistor_238 (.in(1'b0), .out(_39), .gate(IR2));
  Pull_Resistor #(.pull(1)) pull_resistor_42 (.node(_41));
  Transistor #(.\type ("n")) transistor_239 (.in(1'b0), .out(_41), .gate(not_4_out));
  Transistor #(.\type ("n")) transistor_240 (.in(1'b0), .out(_41), .gate(not_6_out));
  Transistor #(.\type ("n")) transistor_241 (.in(1'b0), .out(_41), .gate(not_8_out));
  Transistor #(.\type ("n")) transistor_242 (.in(1'b0), .out(_41), .gate(IR3));
  Transistor #(.\type ("n")) transistor_243 (.in(1'b0), .out(_41), .gate(IR2));
  Pull_Resistor #(.pull(1)) pull_resistor_43 (.node(_42));
  Transistor #(.\type ("n")) transistor_244 (.in(1'b0), .out(_42), .gate(not_3_out));
  Transistor #(.\type ("n")) transistor_245 (.in(1'b0), .out(_42), .gate(not_8_out));
  Transistor #(.\type ("n")) transistor_246 (.in(1'b0), .out(_42), .gate(not_9_out));
  Pull_Resistor #(.pull(1)) pull_resistor_44 (.node(_44));
  Pull_Resistor #(.pull(1)) pull_resistor_45 (.node(_43));
  Transistor #(.\type ("n")) transistor_247 (.in(1'b0), .out(_44), .gate(not_5_out));
  Transistor #(.\type ("n")) transistor_248 (.in(1'b0), .out(_43), .gate(or_1_out));
  Transistor #(.\type ("n")) transistor_249 (.in(1'b0), .out(_43), .gate(IR7));
  Transistor #(.\type ("n")) transistor_250 (.in(1'b0), .out(_44), .gate(not_7_out));
  Transistor #(.\type ("n")) transistor_251 (.in(1'b0), .out(_43), .gate(IR4));
  Transistor #(.\type ("n")) transistor_252 (.in(1'b0), .out(_43), .gate(not_9_out));
  Transistor #(.\type ("n")) transistor_253 (.in(1'b0), .out(_43), .gate(IR2));
  Transistor #(.\type ("n")) transistor_254 (.in(1'b0), .out(_44), .gate(not_11_out));
  Transistor #(.\type ("n")) transistor_255 (.in(1'b0), .out(_44), .gate(not_12_out));
  Transistor #(.\type ("n")) transistor_256 (.in(1'b0), .out(_43), .gate(not_12_out));
  Pull_Resistor #(.pull(1)) pull_resistor_46 (.node(_45));
  Transistor #(.\type ("n")) transistor_257 (.in(1'b0), .out(_45), .gate(not_2_out));
  Transistor #(.\type ("n")) transistor_258 (.in(1'b0), .out(_45), .gate(not_6_out));
  Transistor #(.\type ("n")) transistor_259 (.in(1'b0), .out(_45), .gate(IR4));
  Transistor #(.\type ("n")) transistor_260 (.in(1'b0), .out(_45), .gate(IR3));
  Transistor #(.\type ("n")) transistor_261 (.in(1'b0), .out(_45), .gate(IR2));
  Pull_Resistor #(.pull(1)) pull_resistor_47 (.node(_46));
  Transistor #(.\type ("n")) transistor_262 (.in(1'b0), .out(_46), .gate(not_3_out));
  Transistor #(.\type ("n")) transistor_263 (.in(1'b0), .out(_46), .gate(not_6_out));
  Transistor #(.\type ("n")) transistor_264 (.in(1'b0), .out(_46), .gate(not_8_out));
  Transistor #(.\type ("n")) transistor_265 (.in(1'b0), .out(_46), .gate(IR3));
  Transistor #(.\type ("n")) transistor_266 (.in(1'b0), .out(_46), .gate(IR2));
  Pull_Resistor #(.pull(1)) pull_resistor_48 (.node(_48));
  Pull_Resistor #(.pull(1)) pull_resistor_49 (.node(_47));
  Transistor #(.\type ("n")) transistor_267 (.in(1'b0), .out(_48), .gate(not_4_out));
  Transistor #(.\type ("n")) transistor_268 (.in(1'b0), .out(_47), .gate(or_1_out));
  Transistor #(.\type ("n")) transistor_269 (.in(1'b0), .out(_48), .gate(or_1_out));
  Transistor #(.\type ("n")) transistor_270 (.in(1'b0), .out(_47), .gate(IR7));
  Transistor #(.\type ("n")) transistor_271 (.in(1'b0), .out(_48), .gate(IR7));
  Transistor #(.\type ("n")) transistor_272 (.in(1'b0), .out(_47), .gate(IR4));
  Transistor #(.\type ("n")) transistor_273 (.in(1'b0), .out(_48), .gate(IR4));
  Transistor #(.\type ("n")) transistor_274 (.in(1'b0), .out(_47), .gate(IR3));
  Transistor #(.\type ("n")) transistor_275 (.in(1'b0), .out(_48), .gate(IR3));
  Transistor #(.\type ("n")) transistor_276 (.in(1'b0), .out(_48), .gate(IR2));
  Transistor #(.\type ("n")) transistor_277 (.in(1'b0), .out(_47), .gate(IR2));
  Transistor #(.\type ("n")) transistor_278 (.in(1'b0), .out(_48), .gate(IR6));
  Transistor #(.\type ("n")) transistor_279 (.in(1'b0), .out(_47), .gate(not_11_out));
  Transistor #(.\type ("n")) transistor_280 (.in(1'b0), .out(_48), .gate(not_12_out));
  Pull_Resistor #(.pull(1)) pull_resistor_50 (.node(_49));
  Transistor #(.\type ("n")) transistor_281 (.in(1'b0), .out(_49), .gate(or_1_out));
  Transistor #(.\type ("n")) transistor_282 (.in(1'b0), .out(_49), .gate(not_7_out));
  Transistor #(.\type ("n")) transistor_283 (.in(1'b0), .out(_49), .gate(IR4));
  Transistor #(.\type ("n")) transistor_284 (.in(1'b0), .out(_49), .gate(not_11_out));
  Transistor #(.\type ("n")) transistor_285 (.in(1'b0), .out(_49), .gate(not_13_out));
  Pull_Resistor #(.pull(1)) pull_resistor_51 (.node(_50));
  Transistor #(.\type ("n")) transistor_286 (.in(1'b0), .out(_50), .gate(not_6_out));
  Transistor #(.\type ("n")) transistor_287 (.in(1'b0), .out(_50), .gate(not_7_out));
  Transistor #(.\type ("n")) transistor_288 (.in(1'b0), .out(_50), .gate(not_11_out));
  Transistor #(.\type ("n")) transistor_289 (.in(1'b0), .out(_50), .gate(IR5));
  Transistor #(.\type ("n")) transistor_290 (.in(1'b0), .out(_50), .gate(not_13_out));
  Pull_Resistor #(.pull(1)) pull_resistor_52 (.node(_51));
  Pull_Resistor #(.pull(1)) pull_resistor_53 (.node(_52));
  Transistor #(.\type ("n")) transistor_291 (.in(1'b0), .out(_52), .gate(not_6_out));
  Transistor #(.\type ("n")) transistor_292 (.in(1'b0), .out(_51), .gate(not_6_out));
  Transistor #(.\type ("n")) transistor_293 (.in(1'b0), .out(_51), .gate(not_7_out));
  Transistor #(.\type ("n")) transistor_294 (.in(1'b0), .out(_52), .gate(not_11_out));
  Transistor #(.\type ("n")) transistor_295 (.in(1'b0), .out(_51), .gate(not_11_out));
  Transistor #(.\type ("n")) transistor_296 (.in(1'b0), .out(_52), .gate(not_12_out));
  Transistor #(.\type ("n")) transistor_297 (.in(1'b0), .out(_51), .gate(not_12_out));
  Transistor #(.\type ("n")) transistor_298 (.in(1'b0), .out(_51), .gate(not_13_out));
  Transistor #(.\type ("n")) transistor_299 (.in(1'b0), .out(_52), .gate(not_13_out));
  Pull_Resistor #(.pull(1)) pull_resistor_54 (.node(_53));
  Transistor #(.\type ("n")) transistor_300 (.in(1'b0), .out(_53), .gate(not_5_out));
  Transistor #(.\type ("n")) transistor_301 (.in(1'b0), .out(_53), .gate(IR7));
  Transistor #(.\type ("n")) transistor_302 (.in(1'b0), .out(_53), .gate(IR6));
  Transistor #(.\type ("n")) transistor_303 (.in(1'b0), .out(_53), .gate(not_12_out));
  Pull_Resistor #(.pull(1)) pull_resistor_55 (.node(_54));
  Transistor #(.\type ("n")) transistor_304 (.in(1'b0), .out(_54), .gate(not_3_out));
  Transistor #(.\type ("n")) transistor_305 (.in(1'b0), .out(_54), .gate(or_1_out));
  Transistor #(.\type ("n")) transistor_306 (.in(1'b0), .out(_54), .gate(IR7));
  Transistor #(.\type ("n")) transistor_307 (.in(1'b0), .out(_54), .gate(IR4));
  Transistor #(.\type ("n")) transistor_308 (.in(1'b0), .out(_54), .gate(not_9_out));
  Transistor #(.\type ("n")) transistor_309 (.in(1'b0), .out(_54), .gate(not_10_out));
  Transistor #(.\type ("n")) transistor_310 (.in(1'b0), .out(_54), .gate(not_11_out));
  Pull_Resistor #(.pull(1)) pull_resistor_56 (.node(_55));
  Pull_Resistor #(.pull(1)) pull_resistor_57 (.node(_56));
  Transistor #(.\type ("n")) transistor_311 (.in(1'b0), .out(_56), .gate(not_1_out));
  Transistor #(.\type ("n")) transistor_312 (.in(1'b0), .out(_55), .gate(not_5_out));
  Transistor #(.\type ("n")) transistor_313 (.in(1'b0), .out(_56), .gate(or_1_out));
  Transistor #(.\type ("n")) transistor_314 (.in(1'b0), .out(_56), .gate(IR7));
  Transistor #(.\type ("n")) transistor_315 (.in(1'b0), .out(_55), .gate(IR7));
  Transistor #(.\type ("n")) transistor_316 (.in(1'b0), .out(_56), .gate(IR4));
  Transistor #(.\type ("n")) transistor_317 (.in(1'b0), .out(_56), .gate(IR3));
  Transistor #(.\type ("n")) transistor_318 (.in(1'b0), .out(_56), .gate(IR2));
  Transistor #(.\type ("n")) transistor_319 (.in(1'b0), .out(_56), .gate(IR6));
  Transistor #(.\type ("n")) transistor_320 (.in(1'b0), .out(_55), .gate(IR6));
  Transistor #(.\type ("n")) transistor_321 (.in(1'b0), .out(_56), .gate(not_12_out));
  Pull_Resistor #(.pull(1)) pull_resistor_58 (.node(_57));
  Transistor #(.\type ("n")) transistor_322 (.in(1'b0), .out(_57), .gate(not_4_out));
  Transistor #(.\type ("n")) transistor_323 (.in(1'b0), .out(_57), .gate(or_1_out));
  Transistor #(.\type ("n")) transistor_324 (.in(1'b0), .out(_57), .gate(IR7));
  Transistor #(.\type ("n")) transistor_325 (.in(1'b0), .out(_57), .gate(IR4));
  Transistor #(.\type ("n")) transistor_326 (.in(1'b0), .out(_57), .gate(IR2));
  Pull_Resistor #(.pull(1)) pull_resistor_59 (.node(_58));
  Transistor #(.\type ("n")) transistor_327 (.in(1'b0), .out(_58), .gate(or_1_out));
  Transistor #(.\type ("n")) transistor_328 (.in(1'b0), .out(_58), .gate(not_7_out));
  Transistor #(.\type ("n")) transistor_329 (.in(1'b0), .out(_58), .gate(not_8_out));
  Transistor #(.\type ("n")) transistor_330 (.in(1'b0), .out(_58), .gate(not_9_out));
  Transistor #(.\type ("n")) transistor_331 (.in(1'b0), .out(_58), .gate(IR2));
  Transistor #(.\type ("n")) transistor_332 (.in(1'b0), .out(_58), .gate(IR6));
  Transistor #(.\type ("n")) transistor_333 (.in(1'b0), .out(_58), .gate(IR5));
  Transistor #(.\type ("n")) transistor_334 (.in(1'b0), .out(_58), .gate(not_13_out));
  Pull_Resistor #(.pull(1)) pull_resistor_60 (.node(_59));
  Pull_Resistor #(.pull(1)) pull_resistor_61 (.node(_60));
  Transistor #(.\type ("n")) transistor_335 (.in(1'b0), .out(_59), .gate(not_6_out));
  Transistor #(.\type ("n")) transistor_336 (.in(1'b0), .out(_60), .gate(not_6_out));
  Transistor #(.\type ("n")) transistor_337 (.in(1'b0), .out(_59), .gate(IR7));
  Transistor #(.\type ("n")) transistor_338 (.in(1'b0), .out(_60), .gate(not_11_out));
  Transistor #(.\type ("n")) transistor_339 (.in(1'b0), .out(_60), .gate(not_12_out));
  Transistor #(.\type ("n")) transistor_340 (.in(1'b0), .out(_59), .gate(not_14_out));
  Transistor #(.\type ("n")) transistor_341 (.in(1'b0), .out(_60), .gate(not_14_out));
  Pull_Resistor #(.pull(1)) pull_resistor_62 (.node(_61));
  Transistor #(.\type ("n")) transistor_342 (.in(1'b0), .out(_61), .gate(not_5_out));
  Transistor #(.\type ("n")) transistor_343 (.in(1'b0), .out(_61), .gate(IR7));
  Transistor #(.\type ("n")) transistor_344 (.in(1'b0), .out(_61), .gate(IR4));
  Transistor #(.\type ("n")) transistor_345 (.in(1'b0), .out(_61), .gate(IR2));
  Transistor #(.\type ("n")) transistor_346 (.in(1'b0), .out(_61), .gate(not_14_out));
  Pull_Resistor #(.pull(1)) pull_resistor_63 (.node(_62));
  Transistor #(.\type ("n")) transistor_347 (.in(1'b0), .out(_62), .gate(not_5_out));
  Transistor #(.\type ("n")) transistor_348 (.in(1'b0), .out(_62), .gate(not_7_out));
  Transistor #(.\type ("n")) transistor_349 (.in(1'b0), .out(_62), .gate(IR4));
  Transistor #(.\type ("n")) transistor_350 (.in(1'b0), .out(_62), .gate(not_9_out));
  Transistor #(.\type ("n")) transistor_351 (.in(1'b0), .out(_62), .gate(IR2));
  Transistor #(.\type ("n")) transistor_352 (.in(1'b0), .out(_62), .gate(IR6));
  Transistor #(.\type ("n")) transistor_353 (.in(1'b0), .out(_62), .gate(IR5));
  Transistor #(.\type ("n")) transistor_354 (.in(1'b0), .out(_62), .gate(not_13_out));
  Pull_Resistor #(.pull(1)) pull_resistor_64 (.node(_64));
  Pull_Resistor #(.pull(1)) pull_resistor_65 (.node(_63));
  Transistor #(.\type ("n")) transistor_355 (.in(1'b0), .out(_63), .gate(or_1_out));
  Transistor #(.\type ("n")) transistor_356 (.in(1'b0), .out(_64), .gate(not_6_out));
  Transistor #(.\type ("n")) transistor_357 (.in(1'b0), .out(_63), .gate(IR7));
  Transistor #(.\type ("n")) transistor_358 (.in(1'b0), .out(_64), .gate(not_7_out));
  Transistor #(.\type ("n")) transistor_359 (.in(1'b0), .out(_63), .gate(IR4));
  Transistor #(.\type ("n")) transistor_360 (.in(1'b0), .out(_63), .gate(not_9_out));
  Transistor #(.\type ("n")) transistor_361 (.in(1'b0), .out(_63), .gate(IR2));
  Transistor #(.\type ("n")) transistor_362 (.in(1'b0), .out(_64), .gate(IR6));
  Transistor #(.\type ("n")) transistor_363 (.in(1'b0), .out(_63), .gate(not_11_out));
  Transistor #(.\type ("n")) transistor_364 (.in(1'b0), .out(_63), .gate(not_12_out));
  Transistor #(.\type ("n")) transistor_365 (.in(1'b0), .out(_64), .gate(not_12_out));
  Transistor #(.\type ("n")) transistor_366 (.in(1'b0), .out(_64), .gate(not_13_out));
  Transistor #(.\type ("n")) transistor_367 (.in(1'b0), .out(_63), .gate(not_13_out));
  Pull_Resistor #(.pull(1)) pull_resistor_66 (.node(_65));
  Transistor #(.\type ("n")) transistor_368 (.in(1'b0), .out(_65), .gate(not_6_out));
  Transistor #(.\type ("n")) transistor_369 (.in(1'b0), .out(_65), .gate(not_13_out));
  Pull_Resistor #(.pull(1)) pull_resistor_67 (.node(_66));
  Transistor #(.\type ("n")) transistor_370 (.in(1'b0), .out(_66), .gate(or_1_out));
  Transistor #(.\type ("n")) transistor_371 (.in(1'b0), .out(_66), .gate(not_7_out));
  Transistor #(.\type ("n")) transistor_372 (.in(1'b0), .out(_66), .gate(IR4));
  Transistor #(.\type ("n")) transistor_373 (.in(1'b0), .out(_66), .gate(not_9_out));
  Transistor #(.\type ("n")) transistor_374 (.in(1'b0), .out(_66), .gate(IR2));
  Transistor #(.\type ("n")) transistor_375 (.in(1'b0), .out(_66), .gate(IR6));
  Transistor #(.\type ("n")) transistor_376 (.in(1'b0), .out(_66), .gate(not_12_out));
  Transistor #(.\type ("n")) transistor_377 (.in(1'b0), .out(_66), .gate(not_13_out));
  Pull_Resistor #(.pull(1)) pull_resistor_68 (.node(_67));
  Pull_Resistor #(.pull(1)) pull_resistor_69 (.node(_68));
  Transistor #(.\type ("n")) transistor_378 (.in(1'b0), .out(_67), .gate(not_5_out));
  Transistor #(.\type ("n")) transistor_379 (.in(1'b0), .out(_68), .gate(not_5_out));
  Transistor #(.\type ("n")) transistor_380 (.in(1'b0), .out(_67), .gate(IR7));
  Transistor #(.\type ("n")) transistor_381 (.in(1'b0), .out(_68), .gate(not_7_out));
  Transistor #(.\type ("n")) transistor_382 (.in(1'b0), .out(_67), .gate(IR4));
  Transistor #(.\type ("n")) transistor_383 (.in(1'b0), .out(_68), .gate(IR4));
  Transistor #(.\type ("n")) transistor_384 (.in(1'b0), .out(_67), .gate(not_9_out));
  Transistor #(.\type ("n")) transistor_385 (.in(1'b0), .out(_68), .gate(not_9_out));
  Transistor #(.\type ("n")) transistor_386 (.in(1'b0), .out(_68), .gate(IR2));
  Transistor #(.\type ("n")) transistor_387 (.in(1'b0), .out(_67), .gate(IR2));
  Transistor #(.\type ("n")) transistor_388 (.in(1'b0), .out(_68), .gate(IR6));
  Transistor #(.\type ("n")) transistor_389 (.in(1'b0), .out(_68), .gate(not_12_out));
  Transistor #(.\type ("n")) transistor_390 (.in(1'b0), .out(_68), .gate(not_13_out));
  Transistor #(.\type ("n")) transistor_391 (.in(1'b0), .out(_67), .gate(not_13_out));
  Pull_Resistor #(.pull(1)) pull_resistor_70 (.node(_69));
  Transistor #(.\type ("n")) transistor_392 (.in(1'b0), .out(_69), .gate(or_1_out));
  Transistor #(.\type ("n")) transistor_393 (.in(1'b0), .out(_69), .gate(IR7));
  Transistor #(.\type ("n")) transistor_394 (.in(1'b0), .out(_69), .gate(IR4));
  Transistor #(.\type ("n")) transistor_395 (.in(1'b0), .out(_69), .gate(not_10_out));
  Transistor #(.\type ("n")) transistor_396 (.in(1'b0), .out(_69), .gate(IR6));
  Transistor #(.\type ("n")) transistor_397 (.in(1'b0), .out(_69), .gate(not_12_out));
  Transistor #(.\type ("n")) transistor_398 (.in(1'b0), .out(_69), .gate(not_13_out));
  Pull_Resistor #(.pull(1)) pull_resistor_71 (.node(_70));
  Transistor #(.\type ("n")) transistor_399 (.in(1'b0), .out(_70), .gate(not_6_out));
  Transistor #(.\type ("n")) transistor_400 (.in(1'b0), .out(_70), .gate(IR7));
  Transistor #(.\type ("n")) transistor_401 (.in(1'b0), .out(_70), .gate(IR6));
  Transistor #(.\type ("n")) transistor_402 (.in(1'b0), .out(_70), .gate(not_12_out));
  Transistor #(.\type ("n")) transistor_403 (.in(1'b0), .out(_70), .gate(not_13_out));
  Pull_Resistor #(.pull(1)) pull_resistor_72 (.node(_72));
  Pull_Resistor #(.pull(1)) pull_resistor_73 (.node(_71));
  Transistor #(.\type ("n")) transistor_404 (.in(1'b0), .out(_72), .gate(not_1_out));
  Transistor #(.\type ("n")) transistor_405 (.in(1'b0), .out(_71), .gate(not_2_out));
  Transistor #(.\type ("n")) transistor_406 (.in(1'b0), .out(_72), .gate(not_6_out));
  Transistor #(.\type ("n")) transistor_407 (.in(1'b0), .out(_71), .gate(not_8_out));
  Transistor #(.\type ("n")) transistor_408 (.in(1'b0), .out(_72), .gate(not_8_out));
  Transistor #(.\type ("n")) transistor_409 (.in(1'b0), .out(_72), .gate(IR3));
  Transistor #(.\type ("n")) transistor_410 (.in(1'b0), .out(_71), .gate(not_9_out));
  Transistor #(.\type ("n")) transistor_411 (.in(1'b0), .out(_72), .gate(IR2));
  Pull_Resistor #(.pull(1)) pull_resistor_74 (.node(_73));
  Transistor #(.\type ("n")) transistor_412 (.in(1'b0), .out(_73), .gate(or_1_out));
  Transistor #(.\type ("n")) transistor_413 (.in(1'b0), .out(_73), .gate(not_8_out));
  Transistor #(.\type ("n")) transistor_414 (.in(1'b0), .out(_73), .gate(IR3));
  Transistor #(.\type ("n")) transistor_415 (.in(1'b0), .out(_73), .gate(IR2));
  Transistor #(.\type ("n")) transistor_416 (.in(1'b0), .out(_73), .gate(not_13_out));
  Pull_Resistor #(.pull(1)) pull_resistor_75 (.node(_74));
  Pull_Resistor #(.pull(1)) pull_resistor_76 (.node(_75));
  Transistor #(.\type ("n")) transistor_417 (.in(1'b0), .out(_74), .gate(not_4_out));
  Transistor #(.\type ("n")) transistor_418 (.in(1'b0), .out(_75), .gate(not_5_out));
  Transistor #(.\type ("n")) transistor_419 (.in(1'b0), .out(_74), .gate(or_1_out));
  Transistor #(.\type ("n")) transistor_420 (.in(1'b0), .out(_74), .gate(IR7));
  Transistor #(.\type ("n")) transistor_421 (.in(1'b0), .out(_75), .gate(IR7));
  Transistor #(.\type ("n")) transistor_422 (.in(1'b0), .out(_74), .gate(IR4));
  Transistor #(.\type ("n")) transistor_423 (.in(1'b0), .out(_75), .gate(IR4));
  Transistor #(.\type ("n")) transistor_424 (.in(1'b0), .out(_74), .gate(not_9_out));
  Transistor #(.\type ("n")) transistor_425 (.in(1'b0), .out(_75), .gate(not_9_out));
  Transistor #(.\type ("n")) transistor_426 (.in(1'b0), .out(_75), .gate(IR2));
  Transistor #(.\type ("n")) transistor_427 (.in(1'b0), .out(_74), .gate(IR2));
  Transistor #(.\type ("n")) transistor_428 (.in(1'b0), .out(_74), .gate(not_11_out));
  Transistor #(.\type ("n")) transistor_429 (.in(1'b0), .out(_75), .gate(not_11_out));
  Transistor #(.\type ("n")) transistor_430 (.in(1'b0), .out(_74), .gate(IR5));
  Transistor #(.\type ("n")) transistor_431 (.in(1'b0), .out(_75), .gate(not_13_out));
  Pull_Resistor #(.pull(1)) pull_resistor_77 (.node(_76));
  Transistor #(.\type ("n")) transistor_432 (.in(1'b0), .out(_76), .gate(not_5_out));
  Transistor #(.\type ("n")) transistor_433 (.in(1'b0), .out(_76), .gate(IR7));
  Transistor #(.\type ("n")) transistor_434 (.in(1'b0), .out(_76), .gate(not_11_out));
  Pull_Resistor #(.pull(1)) pull_resistor_78 (.node(_77));
  Transistor #(.\type ("n")) transistor_435 (.in(1'b0), .out(_77), .gate(not_4_out));
  Transistor #(.\type ("n")) transistor_436 (.in(1'b0), .out(_77), .gate(or_1_out));
  Transistor #(.\type ("n")) transistor_437 (.in(1'b0), .out(_77), .gate(IR7));
  Transistor #(.\type ("n")) transistor_438 (.in(1'b0), .out(_77), .gate(IR4));
  Transistor #(.\type ("n")) transistor_439 (.in(1'b0), .out(_77), .gate(IR3));
  Transistor #(.\type ("n")) transistor_440 (.in(1'b0), .out(_77), .gate(IR2));
  Transistor #(.\type ("n")) transistor_441 (.in(1'b0), .out(_77), .gate(IR6));
  Transistor #(.\type ("n")) transistor_442 (.in(1'b0), .out(_77), .gate(IR5));
  Pull_Resistor #(.pull(1)) pull_resistor_79 (.node(_78));
  Pull_Resistor #(.pull(1)) pull_resistor_80 (.node(_79));
  Transistor #(.\type ("n")) transistor_443 (.in(1'b0), .out(_78), .gate(not_3_out));
  Transistor #(.\type ("n")) transistor_444 (.in(1'b0), .out(_78), .gate(or_1_out));
  Transistor #(.\type ("n")) transistor_445 (.in(1'b0), .out(_79), .gate(not_6_out));
  Transistor #(.\type ("n")) transistor_446 (.in(1'b0), .out(_78), .gate(IR7));
  Transistor #(.\type ("n")) transistor_447 (.in(1'b0), .out(_79), .gate(not_7_out));
  Transistor #(.\type ("n")) transistor_448 (.in(1'b0), .out(_78), .gate(IR4));
  Transistor #(.\type ("n")) transistor_449 (.in(1'b0), .out(_78), .gate(IR3));
  Transistor #(.\type ("n")) transistor_450 (.in(1'b0), .out(_78), .gate(IR2));
  Transistor #(.\type ("n")) transistor_451 (.in(1'b0), .out(_79), .gate(IR6));
  Transistor #(.\type ("n")) transistor_452 (.in(1'b0), .out(_78), .gate(IR6));
  Transistor #(.\type ("n")) transistor_453 (.in(1'b0), .out(_79), .gate(IR5));
  Transistor #(.\type ("n")) transistor_454 (.in(1'b0), .out(_78), .gate(not_12_out));
  Pull_Resistor #(.pull(1)) pull_resistor_81 (.node(_80));
  Transistor #(.\type ("n")) transistor_455 (.in(1'b0), .out(_80), .gate(not_4_out));
  Transistor #(.\type ("n")) transistor_456 (.in(1'b0), .out(_80), .gate(or_1_out));
  Transistor #(.\type ("n")) transistor_457 (.in(1'b0), .out(_80), .gate(not_8_out));
  Transistor #(.\type ("n")) transistor_458 (.in(1'b0), .out(_80), .gate(IR3));
  Transistor #(.\type ("n")) transistor_459 (.in(1'b0), .out(_80), .gate(IR2));
  Pull_Resistor #(.pull(1)) pull_resistor_82 (.node(_81));
  Transistor #(.\type ("n")) transistor_460 (.in(1'b0), .out(_81), .gate(not_4_out));
  Transistor #(.\type ("n")) transistor_461 (.in(1'b0), .out(_81), .gate(IR3));
  Transistor #(.\type ("n")) transistor_462 (.in(1'b0), .out(_81), .gate(not_10_out));
  Pull_Resistor #(.pull(1)) pull_resistor_83 (.node(_83));
  Pull_Resistor #(.pull(1)) pull_resistor_84 (.node(_82));
  Transistor #(.\type ("n")) transistor_463 (.in(1'b0), .out(_82), .gate(not_4_out));
  Transistor #(.\type ("n")) transistor_464 (.in(1'b0), .out(_83), .gate(not_4_out));
  Transistor #(.\type ("n")) transistor_465 (.in(1'b0), .out(_82), .gate(not_6_out));
  Transistor #(.\type ("n")) transistor_466 (.in(1'b0), .out(_82), .gate(IR3));
  Transistor #(.\type ("n")) transistor_467 (.in(1'b0), .out(_83), .gate(not_9_out));
  Transistor #(.\type ("n")) transistor_468 (.in(1'b0), .out(_82), .gate(IR2));
  Pull_Resistor #(.pull(1)) pull_resistor_85 (.node(_84));
  Transistor #(.\type ("n")) transistor_469 (.in(1'b0), .out(_84), .gate(not_1_out));
  Transistor #(.\type ("n")) transistor_470 (.in(1'b0), .out(_84), .gate(or_1_out));
  Transistor #(.\type ("n")) transistor_471 (.in(1'b0), .out(_84), .gate(IR7));
  Transistor #(.\type ("n")) transistor_472 (.in(1'b0), .out(_84), .gate(IR4));
  Transistor #(.\type ("n")) transistor_473 (.in(1'b0), .out(_84), .gate(IR3));
  Transistor #(.\type ("n")) transistor_474 (.in(1'b0), .out(_84), .gate(IR2));
  Transistor #(.\type ("n")) transistor_475 (.in(1'b0), .out(_84), .gate(not_11_out));
  Transistor #(.\type ("n")) transistor_476 (.in(1'b0), .out(_84), .gate(not_12_out));
  Pull_Resistor #(.pull(1)) pull_resistor_86 (.node(_85));
  Transistor #(.\type ("n")) transistor_477 (.in(1'b0), .out(_85), .gate(not_2_out));
  Pull_Resistor #(.pull(1)) pull_resistor_87 (.node(_86));
  Pull_Resistor #(.pull(1)) pull_resistor_88 (.node(_87));
  Transistor #(.\type ("n")) transistor_478 (.in(1'b0), .out(_86), .gate(not_3_out));
  Transistor #(.\type ("n")) transistor_479 (.in(1'b0), .out(_87), .gate(or_1_out));
  Transistor #(.\type ("n")) transistor_480 (.in(1'b0), .out(_87), .gate(IR7));
  Transistor #(.\type ("n")) transistor_481 (.in(1'b0), .out(_87), .gate(IR4));
  Transistor #(.\type ("n")) transistor_482 (.in(1'b0), .out(_87), .gate(IR3));
  Transistor #(.\type ("n")) transistor_483 (.in(1'b0), .out(_87), .gate(IR2));
  Transistor #(.\type ("n")) transistor_484 (.in(1'b0), .out(_87), .gate(IR5));
  Transistor #(.\type ("n")) transistor_485 (.in(1'b0), .out(_87), .gate(not_13_out));
  Pull_Resistor #(.pull(1)) pull_resistor_89 (.node(_88));
  Transistor #(.\type ("n")) transistor_486 (.in(1'b0), .out(_88), .gate(or_1_out));
  Transistor #(.\type ("n")) transistor_487 (.in(1'b0), .out(_88), .gate(IR7));
  Transistor #(.\type ("n")) transistor_488 (.in(1'b0), .out(_88), .gate(IR4));
  Transistor #(.\type ("n")) transistor_489 (.in(1'b0), .out(_88), .gate(not_9_out));
  Transistor #(.\type ("n")) transistor_490 (.in(1'b0), .out(_88), .gate(not_10_out));
  Transistor #(.\type ("n")) transistor_491 (.in(1'b0), .out(_88), .gate(not_11_out));
  Transistor #(.\type ("n")) transistor_492 (.in(1'b0), .out(_88), .gate(not_13_out));
  Pull_Resistor #(.pull(1)) pull_resistor_90 (.node(_89));
  Transistor #(.\type ("n")) transistor_493 (.in(1'b0), .out(_89), .gate(not_1_out));
  Transistor #(.\type ("n")) transistor_494 (.in(1'b0), .out(_89), .gate(not_6_out));
  Transistor #(.\type ("n")) transistor_495 (.in(1'b0), .out(_89), .gate(IR4));
  Transistor #(.\type ("n")) transistor_496 (.in(1'b0), .out(_89), .gate(IR3));
  Transistor #(.\type ("n")) transistor_497 (.in(1'b0), .out(_89), .gate(IR2));
  Pull_Resistor #(.pull(1)) pull_resistor_91 (.node(_90));
  Transistor #(.\type ("n")) transistor_498 (.in(1'b0), .out(_90), .gate(not_3_out));
  Transistor #(.\type ("n")) transistor_499 (.in(1'b0), .out(_90), .gate(not_9_out));
  Pull_Resistor #(.pull(1)) pull_resistor_92 (.node(_91));
  Transistor #(.\type ("n")) transistor_500 (.in(1'b0), .out(_91), .gate(not_2_out));
  Transistor #(.\type ("n")) transistor_501 (.in(1'b0), .out(_91), .gate(not_6_out));
  Transistor #(.\type ("n")) transistor_502 (.in(1'b0), .out(_91), .gate(not_8_out));
  Transistor #(.\type ("n")) transistor_503 (.in(1'b0), .out(_91), .gate(IR3));
  Transistor #(.\type ("n")) transistor_504 (.in(1'b0), .out(_91), .gate(IR2));
  Pull_Resistor #(.pull(1)) pull_resistor_93 (.node(_92));
  Transistor #(.\type ("n")) transistor_505 (.in(1'b0), .out(_92), .gate(not_3_out));
  Transistor #(.\type ("n")) transistor_506 (.in(1'b0), .out(_92), .gate(not_8_out));
  Transistor #(.\type ("n")) transistor_507 (.in(1'b0), .out(_92), .gate(not_9_out));
  Pull_Resistor #(.pull(1)) pull_resistor_94 (.node(_94));
  Pull_Resistor #(.pull(1)) pull_resistor_95 (.node(_93));
  Transistor #(.\type ("n")) transistor_508 (.in(1'b0), .out(_93), .gate(not_3_out));
  Transistor #(.\type ("n")) transistor_509 (.in(1'b0), .out(_94), .gate(or_1_out));
  Transistor #(.\type ("n")) transistor_510 (.in(1'b0), .out(_93), .gate(or_1_out));
  Transistor #(.\type ("n")) transistor_511 (.in(1'b0), .out(_94), .gate(IR7));
  Transistor #(.\type ("n")) transistor_512 (.in(1'b0), .out(_94), .gate(IR4));
  Transistor #(.\type ("n")) transistor_513 (.in(1'b0), .out(_93), .gate(not_8_out));
  Transistor #(.\type ("n")) transistor_514 (.in(1'b0), .out(_94), .gate(IR3));
  Transistor #(.\type ("n")) transistor_515 (.in(1'b0), .out(_93), .gate(IR3));
  Transistor #(.\type ("n")) transistor_516 (.in(1'b0), .out(_94), .gate(IR2));
  Transistor #(.\type ("n")) transistor_517 (.in(1'b0), .out(_93), .gate(IR2));
  Transistor #(.\type ("n")) transistor_518 (.in(1'b0), .out(_94), .gate(IR5));
  Pull_Resistor #(.pull(1)) pull_resistor_96 (.node(_95));
  Transistor #(.\type ("n")) transistor_519 (.in(1'b0), .out(_95), .gate(or_1_out));
  Transistor #(.\type ("n")) transistor_520 (.in(1'b0), .out(_95), .gate(IR7));
  Transistor #(.\type ("n")) transistor_521 (.in(1'b0), .out(_95), .gate(IR4));
  Transistor #(.\type ("n")) transistor_522 (.in(1'b0), .out(_95), .gate(IR3));
  Transistor #(.\type ("n")) transistor_523 (.in(1'b0), .out(_95), .gate(IR2));
  Transistor #(.\type ("n")) transistor_524 (.in(1'b0), .out(_95), .gate(IR6));
  Transistor #(.\type ("n")) transistor_525 (.in(1'b0), .out(_95), .gate(not_12_out));
  Pull_Resistor #(.pull(1)) pull_resistor_97 (.node(_96));
  Transistor #(.\type ("n")) transistor_526 (.in(1'b0), .out(_96), .gate(or_1_out));
  Transistor #(.\type ("n")) transistor_527 (.in(1'b0), .out(_96), .gate(IR7));
  Transistor #(.\type ("n")) transistor_528 (.in(1'b0), .out(_96), .gate(IR4));
  Transistor #(.\type ("n")) transistor_529 (.in(1'b0), .out(_96), .gate(not_9_out));
  Transistor #(.\type ("n")) transistor_530 (.in(1'b0), .out(_96), .gate(not_10_out));
  Transistor #(.\type ("n")) transistor_531 (.in(1'b0), .out(_96), .gate(not_11_out));
  Pull_Resistor #(.pull(1)) pull_resistor_98 (.node(_97));
  Transistor #(.\type ("n")) transistor_532 (.in(1'b0), .out(_97), .gate(not_7_out));
  Transistor #(.\type ("n")) transistor_533 (.in(1'b0), .out(_97), .gate(IR6));
  Transistor #(.\type ("n")) transistor_534 (.in(1'b0), .out(_97), .gate(IR5));
  Pull_Resistor #(.pull(1)) pull_resistor_99 (.node(_98));
  Transistor #(.\type ("n")) transistor_535 (.in(1'b0), .out(_98), .gate(not_2_out));
  Transistor #(.\type ("n")) transistor_536 (.in(1'b0), .out(_98), .gate(or_1_out));
  Transistor #(.\type ("n")) transistor_537 (.in(1'b0), .out(_98), .gate(IR7));
  Transistor #(.\type ("n")) transistor_538 (.in(1'b0), .out(_98), .gate(IR4));
  Transistor #(.\type ("n")) transistor_539 (.in(1'b0), .out(_98), .gate(IR3));
  Transistor #(.\type ("n")) transistor_540 (.in(1'b0), .out(_98), .gate(IR2));
  Transistor #(.\type ("n")) transistor_541 (.in(1'b0), .out(_98), .gate(IR6));
  Transistor #(.\type ("n")) transistor_542 (.in(1'b0), .out(_98), .gate(IR5));
  Pull_Resistor #(.pull(1)) pull_resistor_100 (.node(_100));
  Pull_Resistor #(.pull(1)) pull_resistor_101 (.node(_99));
  Transistor #(.\type ("n")) transistor_543 (.in(1'b0), .out(_99), .gate(not_4_out));
  Transistor #(.\type ("n")) transistor_544 (.in(1'b0), .out(_100), .gate(not_4_out));
  Transistor #(.\type ("n")) transistor_545 (.in(1'b0), .out(_100), .gate(or_1_out));
  Transistor #(.\type ("n")) transistor_546 (.in(1'b0), .out(_99), .gate(or_1_out));
  Transistor #(.\type ("n")) transistor_547 (.in(1'b0), .out(_99), .gate(IR7));
  Transistor #(.\type ("n")) transistor_548 (.in(1'b0), .out(_100), .gate(IR7));
  Transistor #(.\type ("n")) transistor_549 (.in(1'b0), .out(_100), .gate(IR4));
  Transistor #(.\type ("n")) transistor_550 (.in(1'b0), .out(_99), .gate(IR4));
  Transistor #(.\type ("n")) transistor_551 (.in(1'b0), .out(_100), .gate(not_9_out));
  Transistor #(.\type ("n")) transistor_552 (.in(1'b0), .out(_99), .gate(not_9_out));
  Transistor #(.\type ("n")) transistor_553 (.in(1'b0), .out(_99), .gate(IR2));
  Transistor #(.\type ("n")) transistor_554 (.in(1'b0), .out(_100), .gate(IR2));
  Transistor #(.\type ("n")) transistor_555 (.in(1'b0), .out(_99), .gate(IR6));
  Transistor #(.\type ("n")) transistor_556 (.in(1'b0), .out(_99), .gate(IR5));
  Transistor #(.\type ("n")) transistor_557 (.in(1'b0), .out(_100), .gate(IR5));
  Pull_Resistor #(.pull(1)) pull_resistor_102 (.node(_101));
  Transistor #(.\type ("n")) transistor_558 (.in(1'b0), .out(_101), .gate(not_2_out));
  Transistor #(.\type ("n")) transistor_559 (.in(1'b0), .out(_101), .gate(or_1_out));
  Transistor #(.\type ("n")) transistor_560 (.in(1'b0), .out(_101), .gate(IR7));
  Transistor #(.\type ("n")) transistor_561 (.in(1'b0), .out(_101), .gate(IR4));
  Transistor #(.\type ("n")) transistor_562 (.in(1'b0), .out(_101), .gate(not_9_out));
  Transistor #(.\type ("n")) transistor_563 (.in(1'b0), .out(_101), .gate(not_10_out));
  Transistor #(.\type ("n")) transistor_564 (.in(1'b0), .out(_101), .gate(not_11_out));
  Pull_Resistor #(.pull(1)) pull_resistor_103 (.node(_102));
  Transistor #(.\type ("n")) transistor_565 (.in(1'b0), .out(_102), .gate(not_1_out));
  Transistor #(.\type ("n")) transistor_566 (.in(1'b0), .out(_102), .gate(or_1_out));
  Transistor #(.\type ("n")) transistor_567 (.in(1'b0), .out(_102), .gate(IR7));
  Transistor #(.\type ("n")) transistor_568 (.in(1'b0), .out(_102), .gate(IR4));
  Transistor #(.\type ("n")) transistor_569 (.in(1'b0), .out(_102), .gate(IR3));
  Transistor #(.\type ("n")) transistor_570 (.in(1'b0), .out(_102), .gate(IR2));
  Transistor #(.\type ("n")) transistor_571 (.in(1'b0), .out(_102), .gate(not_11_out));
  Pull_Resistor #(.pull(1)) pull_resistor_104 (.node(_103));
  Transistor #(.\type ("n")) transistor_572 (.in(1'b0), .out(_103), .gate(not_1_out));
  Transistor #(.\type ("n")) transistor_573 (.in(1'b0), .out(_103), .gate(or_1_out));
  Transistor #(.\type ("n")) transistor_574 (.in(1'b0), .out(_103), .gate(IR7));
  Transistor #(.\type ("n")) transistor_575 (.in(1'b0), .out(_103), .gate(IR4));
  Transistor #(.\type ("n")) transistor_576 (.in(1'b0), .out(_103), .gate(IR3));
  Transistor #(.\type ("n")) transistor_577 (.in(1'b0), .out(_103), .gate(IR2));
  Transistor #(.\type ("n")) transistor_578 (.in(1'b0), .out(_103), .gate(IR6));
  Transistor #(.\type ("n")) transistor_579 (.in(1'b0), .out(_103), .gate(not_12_out));
  Pull_Resistor #(.pull(1)) pull_resistor_105 (.node(_104));
  Pull_Resistor #(.pull(1)) pull_resistor_106 (.node(_105));
  Transistor #(.\type ("n")) transistor_580 (.in(1'b0), .out(_105), .gate(not_3_out));
  Transistor #(.\type ("n")) transistor_581 (.in(1'b0), .out(_104), .gate(not_4_out));
  Transistor #(.\type ("n")) transistor_582 (.in(1'b0), .out(_104), .gate(or_1_out));
  Transistor #(.\type ("n")) transistor_583 (.in(1'b0), .out(_105), .gate(or_1_out));
  Transistor #(.\type ("n")) transistor_584 (.in(1'b0), .out(_104), .gate(IR7));
  Transistor #(.\type ("n")) transistor_585 (.in(1'b0), .out(_105), .gate(IR7));
  Transistor #(.\type ("n")) transistor_586 (.in(1'b0), .out(_104), .gate(IR4));
  Transistor #(.\type ("n")) transistor_587 (.in(1'b0), .out(_105), .gate(IR4));
  Transistor #(.\type ("n")) transistor_588 (.in(1'b0), .out(_105), .gate(not_9_out));
  Transistor #(.\type ("n")) transistor_589 (.in(1'b0), .out(_104), .gate(not_9_out));
  Transistor #(.\type ("n")) transistor_590 (.in(1'b0), .out(_105), .gate(IR2));
  Transistor #(.\type ("n")) transistor_591 (.in(1'b0), .out(_104), .gate(not_10_out));
  Transistor #(.\type ("n")) transistor_592 (.in(1'b0), .out(_104), .gate(not_11_out));
  Transistor #(.\type ("n")) transistor_593 (.in(1'b0), .out(_104), .gate(IR5));
  Transistor #(.\type ("n")) transistor_594 (.in(1'b0), .out(_105), .gate(not_12_out));
  Pull_Resistor #(.pull(1)) pull_resistor_107 (.node(_106));
  Transistor #(.\type ("n")) transistor_595 (.in(1'b0), .out(_106), .gate(not_5_out));
  Transistor #(.\type ("n")) transistor_596 (.in(1'b0), .out(_106), .gate(not_11_out));
  Pull_Resistor #(.pull(1)) pull_resistor_108 (.node(_107));
  Transistor #(.\type ("n")) transistor_597 (.in(1'b0), .out(_107), .gate(not_5_out));
  Transistor #(.\type ("n")) transistor_598 (.in(1'b0), .out(_107), .gate(IR7));
  Transistor #(.\type ("n")) transistor_599 (.in(1'b0), .out(_107), .gate(IR6));
  Pull_Resistor #(.pull(1)) pull_resistor_109 (.node(_108));
  Transistor #(.\type ("n")) transistor_600 (.in(1'b0), .out(_108), .gate(or_1_out));
  Transistor #(.\type ("n")) transistor_601 (.in(1'b0), .out(_108), .gate(IR7));
  Transistor #(.\type ("n")) transistor_602 (.in(1'b0), .out(_108), .gate(not_8_out));
  Transistor #(.\type ("n")) transistor_603 (.in(1'b0), .out(_108), .gate(IR2));
  Transistor #(.\type ("n")) transistor_604 (.in(1'b0), .out(_108), .gate(not_11_out));
  Transistor #(.\type ("n")) transistor_605 (.in(1'b0), .out(_108), .gate(not_13_out));
  Pull_Resistor #(.pull(1)) pull_resistor_110 (.node(_109));
  Transistor #(.\type ("n")) transistor_606 (.in(1'b0), .out(_109), .gate(or_1_out));
  Transistor #(.\type ("n")) transistor_607 (.in(1'b0), .out(_109), .gate(IR7));
  Transistor #(.\type ("n")) transistor_608 (.in(1'b0), .out(_109), .gate(IR4));
  Transistor #(.\type ("n")) transistor_609 (.in(1'b0), .out(_109), .gate(not_10_out));
  Transistor #(.\type ("n")) transistor_610 (.in(1'b0), .out(_109), .gate(IR6));
  Transistor #(.\type ("n")) transistor_611 (.in(1'b0), .out(_109), .gate(not_12_out));
  Transistor #(.\type ("n")) transistor_612 (.in(1'b0), .out(_109), .gate(not_14_out));
  Pull_Resistor #(.pull(1)) pull_resistor_111 (.node(_111));
  Pull_Resistor #(.pull(1)) pull_resistor_112 (.node(_110));
  Transistor #(.\type ("n")) transistor_613 (.in(1'b0), .out(_111), .gate(not_3_out));
  Transistor #(.\type ("n")) transistor_614 (.in(1'b0), .out(_110), .gate(or_1_out));
  Transistor #(.\type ("n")) transistor_615 (.in(1'b0), .out(_110), .gate(IR7));
  Transistor #(.\type ("n")) transistor_616 (.in(1'b0), .out(_110), .gate(not_8_out));
  Transistor #(.\type ("n")) transistor_617 (.in(1'b0), .out(_111), .gate(not_8_out));
  Transistor #(.\type ("n")) transistor_618 (.in(1'b0), .out(_111), .gate(IR3));
  Transistor #(.\type ("n")) transistor_619 (.in(1'b0), .out(_110), .gate(not_9_out));
  Transistor #(.\type ("n")) transistor_620 (.in(1'b0), .out(_110), .gate(IR2));
  Transistor #(.\type ("n")) transistor_621 (.in(1'b0), .out(_111), .gate(not_10_out));
  Transistor #(.\type ("n")) transistor_622 (.in(1'b0), .out(_110), .gate(IR6));
  Transistor #(.\type ("n")) transistor_623 (.in(1'b0), .out(_110), .gate(not_13_out));
  Pull_Resistor #(.pull(1)) pull_resistor_113 (.node(_112));
  Transistor #(.\type ("n")) transistor_624 (.in(1'b0), .out(_112), .gate(not_6_out));
  Transistor #(.\type ("n")) transistor_625 (.in(1'b0), .out(_112), .gate(not_11_out));
  Transistor #(.\type ("n")) transistor_626 (.in(1'b0), .out(_112), .gate(not_12_out));
  Transistor #(.\type ("n")) transistor_627 (.in(1'b0), .out(_112), .gate(not_14_out));
  Pull_Resistor #(.pull(1)) pull_resistor_114 (.node(_113));
  Transistor #(.\type ("n")) transistor_628 (.in(1'b0), .out(_113), .gate(or_1_out));
  Transistor #(.\type ("n")) transistor_629 (.in(1'b0), .out(_113), .gate(IR7));
  Transistor #(.\type ("n")) transistor_630 (.in(1'b0), .out(_113), .gate(IR4));
  Transistor #(.\type ("n")) transistor_631 (.in(1'b0), .out(_113), .gate(not_10_out));
  Transistor #(.\type ("n")) transistor_632 (.in(1'b0), .out(_113), .gate(IR6));
  Transistor #(.\type ("n")) transistor_633 (.in(1'b0), .out(_113), .gate(not_12_out));
  Transistor #(.\type ("n")) transistor_634 (.in(1'b0), .out(_113), .gate(not_13_out));
  Pull_Resistor #(.pull(1)) pull_resistor_115 (.node(_115));
  Pull_Resistor #(.pull(1)) pull_resistor_116 (.node(_114));
  Transistor #(.\type ("n")) transistor_635 (.in(1'b0), .out(_115), .gate(not_2_out));
  Transistor #(.\type ("n")) transistor_636 (.in(1'b0), .out(_114), .gate(or_1_out));
  Transistor #(.\type ("n")) transistor_637 (.in(1'b0), .out(_115), .gate(or_1_out));
  Transistor #(.\type ("n")) transistor_638 (.in(1'b0), .out(_115), .gate(IR7));
  Transistor #(.\type ("n")) transistor_639 (.in(1'b0), .out(_114), .gate(IR7));
  Transistor #(.\type ("n")) transistor_640 (.in(1'b0), .out(_115), .gate(IR4));
  Transistor #(.\type ("n")) transistor_641 (.in(1'b0), .out(_114), .gate(IR4));
  Transistor #(.\type ("n")) transistor_642 (.in(1'b0), .out(_115), .gate(IR3));
  Transistor #(.\type ("n")) transistor_643 (.in(1'b0), .out(_114), .gate(not_9_out));
  Transistor #(.\type ("n")) transistor_644 (.in(1'b0), .out(_114), .gate(IR2));
  Transistor #(.\type ("n")) transistor_645 (.in(1'b0), .out(_115), .gate(IR2));
  Transistor #(.\type ("n")) transistor_646 (.in(1'b0), .out(_114), .gate(IR6));
  Transistor #(.\type ("n")) transistor_647 (.in(1'b0), .out(_115), .gate(not_11_out));
  Transistor #(.\type ("n")) transistor_648 (.in(1'b0), .out(_115), .gate(IR5));
  Transistor #(.\type ("n")) transistor_649 (.in(1'b0), .out(_114), .gate(not_12_out));
  Transistor #(.\type ("n")) transistor_650 (.in(1'b0), .out(_114), .gate(not_13_out));
  Pull_Resistor #(.pull(1)) pull_resistor_117 (.node(_116));
  Transistor #(.\type ("n")) transistor_651 (.in(1'b0), .out(_116), .gate(not_6_out));
  Transistor #(.\type ("n")) transistor_652 (.in(1'b0), .out(_116), .gate(not_7_out));
  Transistor #(.\type ("n")) transistor_653 (.in(1'b0), .out(_116), .gate(not_11_out));
  Transistor #(.\type ("n")) transistor_654 (.in(1'b0), .out(_116), .gate(IR5));
  Transistor #(.\type ("n")) transistor_655 (.in(1'b0), .out(_116), .gate(not_14_out));
  Pull_Resistor #(.pull(1)) pull_resistor_118 (.node(_117));
  Transistor #(.\type ("n")) transistor_656 (.in(1'b0), .out(_117), .gate(or_1_out));
  Transistor #(.\type ("n")) transistor_657 (.in(1'b0), .out(_117), .gate(not_7_out));
  Transistor #(.\type ("n")) transistor_658 (.in(1'b0), .out(_117), .gate(IR4));
  Transistor #(.\type ("n")) transistor_659 (.in(1'b0), .out(_117), .gate(not_9_out));
  Transistor #(.\type ("n")) transistor_660 (.in(1'b0), .out(_117), .gate(not_10_out));
  Transistor #(.\type ("n")) transistor_661 (.in(1'b0), .out(_117), .gate(not_11_out));
  Transistor #(.\type ("n")) transistor_662 (.in(1'b0), .out(_117), .gate(not_14_out));
  Pull_Resistor #(.pull(1)) pull_resistor_119 (.node(_118));
  Pull_Resistor #(.pull(1)) pull_resistor_120 (.node(_119));
  Transistor #(.\type ("n")) transistor_663 (.in(1'b0), .out(_118), .gate(not_5_out));
  Transistor #(.\type ("n")) transistor_664 (.in(1'b0), .out(_119), .gate(or_1_out));
  Transistor #(.\type ("n")) transistor_665 (.in(1'b0), .out(_118), .gate(IR7));
  Transistor #(.\type ("n")) transistor_666 (.in(1'b0), .out(_119), .gate(not_7_out));
  Transistor #(.\type ("n")) transistor_667 (.in(1'b0), .out(_118), .gate(IR4));
  Transistor #(.\type ("n")) transistor_668 (.in(1'b0), .out(_119), .gate(IR4));
  Transistor #(.\type ("n")) transistor_669 (.in(1'b0), .out(_119), .gate(IR3));
  Transistor #(.\type ("n")) transistor_670 (.in(1'b0), .out(_118), .gate(not_9_out));
  Transistor #(.\type ("n")) transistor_671 (.in(1'b0), .out(_118), .gate(IR2));
  Transistor #(.\type ("n")) transistor_672 (.in(1'b0), .out(_118), .gate(IR6));
  Transistor #(.\type ("n")) transistor_673 (.in(1'b0), .out(_119), .gate(not_11_out));
  Transistor #(.\type ("n")) transistor_674 (.in(1'b0), .out(_119), .gate(not_14_out));
  Transistor #(.\type ("n")) transistor_675 (.in(1'b0), .out(_118), .gate(not_14_out));
  Pull_Resistor #(.pull(1)) pull_resistor_121 (.node(_121));
  Pull_Resistor #(.pull(1)) pull_resistor_122 (.node(_120));
  Transistor #(.\type ("n")) transistor_676 (.in(1'b0), .out(_120), .gate(or_1_out));
  Transistor #(.\type ("n")) transistor_677 (.in(1'b0), .out(_120), .gate(not_7_out));
  Transistor #(.\type ("n")) transistor_678 (.in(1'b0), .out(_120), .gate(not_8_out));
  Transistor #(.\type ("n")) transistor_679 (.in(1'b0), .out(_120), .gate(not_9_out));
  Transistor #(.\type ("n")) transistor_680 (.in(1'b0), .out(_120), .gate(IR2));
  Transistor #(.\type ("n")) transistor_681 (.in(1'b0), .out(_121), .gate(IR6));
  Transistor #(.\type ("n")) transistor_682 (.in(1'b0), .out(_120), .gate(not_11_out));
  Transistor #(.\type ("n")) transistor_683 (.in(1'b0), .out(_120), .gate(not_13_out));
  Pull_Resistor #(.pull(1)) pull_resistor_123 (.node(_122));
  Transistor #(.\type ("n")) transistor_684 (.in(1'b0), .out(_122), .gate(not_3_out));
  Transistor #(.\type ("n")) transistor_685 (.in(1'b0), .out(_122), .gate(IR4));
  Transistor #(.\type ("n")) transistor_686 (.in(1'b0), .out(_122), .gate(not_9_out));
  Transistor #(.\type ("n")) transistor_687 (.in(1'b0), .out(_122), .gate(not_10_out));
  Pull_Resistor #(.pull(1)) pull_resistor_124 (.node(_123));
  Transistor #(.\type ("n")) transistor_688 (.in(1'b0), .out(_123), .gate(not_4_out));
  Transistor #(.\type ("n")) transistor_689 (.in(1'b0), .out(_123), .gate(IR4));
  Transistor #(.\type ("n")) transistor_690 (.in(1'b0), .out(_123), .gate(IR3));
  Transistor #(.\type ("n")) transistor_691 (.in(1'b0), .out(_123), .gate(not_10_out));
  Pull_Resistor #(.pull(1)) pull_resistor_125 (.node(_125));
  Pull_Resistor #(.pull(1)) pull_resistor_126 (.node(_124));
  Transistor #(.\type ("n")) transistor_692 (.in(1'b0), .out(_124), .gate(not_1_out));
  Transistor #(.\type ("n")) transistor_693 (.in(1'b0), .out(_125), .gate(not_2_out));
  Transistor #(.\type ("n")) transistor_694 (.in(1'b0), .out(_124), .gate(not_6_out));
  Transistor #(.\type ("n")) transistor_695 (.in(1'b0), .out(_125), .gate(not_8_out));
  Transistor #(.\type ("n")) transistor_696 (.in(1'b0), .out(_124), .gate(IR3));
  Transistor #(.\type ("n")) transistor_697 (.in(1'b0), .out(_125), .gate(not_9_out));
  Transistor #(.\type ("n")) transistor_698 (.in(1'b0), .out(_124), .gate(IR2));
  Pull_Resistor #(.pull(1)) pull_resistor_127 (.node(_126));
  Transistor #(.\type ("n")) transistor_699 (.in(1'b0), .out(_126), .gate(IR7));
  Pull_Resistor #(.pull(1)) pull_resistor_128 (.node(_127));
  Transistor #(.\type ("n")) transistor_700 (.in(1'b0), .out(_127), .gate(or_1_out));
  Transistor #(.\type ("n")) transistor_701 (.in(1'b0), .out(_127), .gate(not_7_out));
  Transistor #(.\type ("n")) transistor_702 (.in(1'b0), .out(_127), .gate(not_8_out));
  Transistor #(.\type ("n")) transistor_703 (.in(1'b0), .out(_127), .gate(not_9_out));
  Transistor #(.\type ("n")) transistor_704 (.in(1'b0), .out(_127), .gate(IR2));
  Transistor #(.\type ("n")) transistor_705 (.in(1'b0), .out(_127), .gate(IR6));
  Transistor #(.\type ("n")) transistor_706 (.in(1'b0), .out(_127), .gate(not_12_out));
  Pull_Resistor #(.pull(1)) pull_resistor_129 (.node(_129));
  Pull_Resistor #(.pull(1)) pull_resistor_130 (.node(_128));
  Transistor #(.\type ("n")) transistor_707 (.in(1'b0), .out(_128), .gate(IR0));
  Transistor #(.\type ("n")) transistor_708 (.in(1'b0), .out(_129), .gate(or_1_out));
  Transistor #(.\type ("n")) transistor_709 (.in(1'b0), .out(_129), .gate(IR7));
  Transistor #(.\type ("n")) transistor_710 (.in(1'b0), .out(_129), .gate(IR4));
  Transistor #(.\type ("n")) transistor_711 (.in(1'b0), .out(_128), .gate(not_9_out));
  Transistor #(.\type ("n")) transistor_712 (.in(1'b0), .out(_129), .gate(not_9_out));
  Transistor #(.\type ("n")) transistor_713 (.in(1'b0), .out(_129), .gate(IR2));
  Transistor #(.\type ("n")) transistor_714 (.in(1'b0), .out(_128), .gate(IR2));
endmodule

module PREDECODE (
  input  PHI2,
  input  _0_IR,
  input  D0,
  input  D1,
  input  D2,
  input  D3,
  input  D4,
  input  D5,
  input  D6,
  input  D7,
  output IMPLIED,
  output TWOCYCLE,
  output PD0,
  output PD1,
  output PD2,
  output PD3,
  output PD4,
  output PD5,
  output PD6,
  output PD7
);

  wire and_9_out, d_latch_1_q, d_latch_2_q, d_latch_3_q, d_latch_4_q, d_latch_5_q, d_latch_6_q, d_latch_7_q,
       d_latch_8_q, nand_1_out, nor_2_out, nor_3_out, nor_4_out, not_1_out, not_2_out, not_3_out, not_4_out,
       not_5_out, or_1_out;

  not not_1 (not_1_out, _0_IR);
  D_latch d_latch_1 (.EN(PHI2), .D(D0), .Q(d_latch_1_q));  // open: NOT_Q
  D_latch d_latch_2 (.EN(PHI2), .D(D1), .Q(d_latch_2_q));  // open: NOT_Q
  D_latch d_latch_3 (.EN(PHI2), .D(D2), .Q(d_latch_3_q));  // open: NOT_Q
  D_latch d_latch_4 (.EN(PHI2), .D(D3), .Q(d_latch_4_q));  // open: NOT_Q
  D_latch d_latch_5 (.EN(PHI2), .D(D4), .Q(d_latch_5_q));  // open: NOT_Q
  D_latch d_latch_6 (.D(D5), .Q(d_latch_6_q));  // open: EN, NOT_Q
  D_latch d_latch_7 (.EN(PHI2), .D(D6), .Q(d_latch_7_q));  // open: NOT_Q
  D_latch d_latch_8 (.EN(PHI2), .D(D7), .Q(d_latch_8_q));  // open: NOT_Q
  and and_1 (PD0, d_latch_1_q, not_1_out);
  and and_2 (PD1, d_latch_2_q, not_1_out);
  and and_3 (PD2, d_latch_3_q, not_1_out);
  and and_4 (PD3, d_latch_4_q, not_1_out);
  and and_5 (PD4, d_latch_5_q, not_1_out);
  and and_6 (PD5, d_latch_6_q, not_1_out);
  and and_7 (PD6, d_latch_7_q, not_1_out);
  and and_8 (PD7, d_latch_8_q, not_1_out);
  not not_2 (not_2_out, PD3);
  nor nor_1 (IMPLIED, PD0, PD2, not_2_out);
  or or_1 (or_1_out, PD1, PD4, PD7);
  not not_3 (not_3_out, PD0);
  not not_4 (not_4_out, PD3);
  nor nor_2 (nor_2_out, not_3_out, PD2, not_4_out, PD4);
  not not_5 (not_5_out, PD7);
  nor nor_3 (nor_3_out, PD0, PD2, PD3, PD4, not_5_out);
  nand nand_1 (nand_1_out, IMPLIED, or_1_out);
  nor nor_4 (nor_4_out, nor_2_out, nor_3_out);
  and and_9 (and_9_out, nand_1_out, nor_4_out);
  not not_6 (TWOCYCLE, and_9_out);
endmodule

module RANDOM_LOGIC (
  input  X0,
  input  X1,
  input  X2,
  input  X3,
  input  X4,
  input  X5,
  input  X6,
  input  X7,
  input  X8,
  input  X9,
  input  X10,
  input  X11,
  input  X12,
  input  X13,
  input  X14,
  input  X15,
  input  X16,
  input  X17,
  input  X18,
  input  X19,
  input  X20,
  input  X21,
  input  X22,
  input  X23,
  input  X24,
  input  X25,
  input  X26,
  input  X27,
  input  X28,
  input  X29,
  input  X30,
  input  X31,
  input  X32,
  input  X33,
  input  X34,
  input  X35,
  input  X36,
  input  X37,
  input  X38,
  input  X39,
  input  X40,
  input  X41,
  input  X42,
  input  X43,
  input  X44,
  input  X45,
  input  X46,
  input  X47,
  input  X48,
  input  X49,
  input  X50,
  input  X51,
  input  X52,
  input  X53,
  input  X54,
  input  X55,
  input  X56,
  input  X57,
  input  X58,
  input  X59,
  input  X60,
  input  X61,
  input  X62,
  input  X63,
  input  X64,
  input  X65,
  input  X66,
  input  X67,
  input  X68,
  input  X69,
  input  X70,
  input  X71,
  input  X72,
  input  X73,
  input  X74,
  input  X75,
  input  X76,
  input  X77,
  input  X78,
  input  X79,
  input  X80,
  input  X81,
  input  X82,
  input  X83,
  input  X84,
  input  X85,
  input  X86,
  input  X87,
  input  X88,
  input  X89,
  input  X90,
  input  X91,
  input  X92,
  input  X93,
  input  X94,
  input  X95,
  input  X96,
  input  X97,
  input  X98,
  input  X99,
  input  X100,
  input  X101,
  input  X102,
  input  X103,
  input  X104,
  input  X105,
  input  X106,
  input  X107,
  input  X108,
  input  X109,
  input  X110,
  input  X111,
  input  X112,
  input  X113,
  input  X114,
  input  X115,
  input  X116,
  input  X117,
  input  X118,
  input  X119,
  input  X120,
  input  X121,
  input  X122,
  input  X123,
  input  X124,
  input  X125,
  input  X126,
  input  X127,
  input  X128,
  input  X129,
  input  PHI1,
  input  NMIP,
  input  PHI2,
  input  IRQP,
  input  RESP,
  input  TWOCYCLE,
  input  IMPLIED,
  input  RDY,
  input  SO,
  input  ACR,
  input  AVR,
  input  DB7,
  input  DB6,
  input  DB5,
  input  DB4,
  input  DB3,
  input  DB2,
  input  DB1,
  input  DB0,
  output FETCH,
  output WR,
  output _0_IR,
  output T0,
  output T1,
  output T2,
  output T3,
  output T4,
  output T5,
  output ADH_ABH,
  output ADL_ABL,
  output Y_SB,
  output X_SB,
  output _0_ADL0,
  output _0_ADL1,
  output _0_ADL2,
  output SB_Y,
  output SB_X,
  output S_SB,
  output S_ADL,
  output SB_S,
  output S_S
);
endmodule

module D_latch (
  input  EN,
  input  D,
  output Q,
  output NOT_Q
);

  D_Flip_Flop #(.trigger("high")) d_ff_1 (.clk(EN), .D(D), .Q(Q), .Qn(NOT_Q));  // open: preset, en, reset
endmodule

module NMI_FF (
  input  nNMI,
  input  PHI2,
  output NMIP
);

  wire and_1_out, and_2_out, nor_1_out, nor_2_out, not_1_out;

  not not_1 (not_1_out, nNMI);
  and and_1 (and_1_out, not_1_out, PHI2);
  nor nor_1 (nor_1_out, and_2_out, nor_2_out);
  and and_2 (and_2_out, nNMI, PHI2);
  nor nor_2 (nor_2_out, nor_1_out, and_1_out);
  not not_2 (NMIP, nor_2_out);
endmodule
