// Logisim project INT.circ as structural Verilog: 2 circuits, main circuit main
module main (
  input  nNMI,
  input  nIRQ,
  input  nRES,
  input  nI_OUT,
  input  BR2,
  input  T0,
  input  BRK5,
  input  nready,
  output _0_ADL0,
  output _0_ADL1,
  output _0_ADL2,
  output DORES,
  output B_OUT
);

  wire and_1_out, and_2_out, and_3_out, and_4_out, and_5_out, and_6_out, and_7_out, and_8_out, and_9_out,
       and_10_out, and_11_out, d_latch_1_out, d_latch_2_out_2, d_latch_3_out_2, d_latch_4_out_2,
       d_latch_5_out_2, d_latch_6_out, d_latch_7_out_2, d_latch_8_out_2, d_latch_9_out, d_latch_10_out,
       d_latch_11_out, d_latch_12_out, d_latch_13_out, d_latch_14_out, d_latch_15_out, d_latch_16_out,
       d_latch_17_out, d_latch_20_out_2, nand_1_out, nand_2_out, nand_3_out, nand_4_out, nand_5_out,
       nand_6_out, nand_7_out, nor_1_out, nor_2_out, nor_3_out, nor_4_out, nor_5_out, nor_6_out, nor_7_out,
       nor_8_out, nor_9_out, nor_10_out, nor_11_out, nor_13_out, not_1_out, not_2_out, not_3_out, not_4_out,
       not_5_out, not_6_out, not_7_out, not_8_out, not_9_out, not_10_out, not_11_out, not_12_out, not_13_out,
       not_14_out, not_15_out, not_16_out, not_17_out, not_18_out, not_19_out, not_20_out, not_21_out,
       not_22_out, not_23_out, not_24_out, not_25_out, not_26_out, not_27_out, not_28_out, not_29_out,
       not_31_out, not_32_out, not_33_out, not_34_out, or_1_out, or_2_out, or_3_out, PHI0_out;

  Clock PHI0 (.out(PHI0_out));
  Transistor #(.\type ("n")) transistor_1 (.in(1'b0), .out(nRES), .gate(1'b0));
  Transistor #(.\type ("n")) transistor_2 (.in(1'b0), .out(nIRQ), .gate(1'b0));
  Transistor #(.\type ("n")) transistor_3 (.in(1'b0), .out(nNMI), .gate(1'b0));
  not not_1 (not_1_out, nNMI);
  not not_2 (not_2_out, nIRQ);
  not not_3 (not_3_out, nRES);
  not not_4 (not_4_out, nready);
  not not_5 (not_5_out, not_1_out);
  not not_6 (not_6_out, not_2_out);
  not not_7 (not_7_out, not_3_out);
  and and_1 (and_1_out, BRK5, not_4_out);
  nand nand_1 (nand_1_out, not_1_out, PHI0_out);
  not not_8 (not_8_out, and_3_out);
  nand nand_2 (nand_2_out, not_5_out, PHI0_out);
  not not_9 (not_9_out, and_2_out);
  nand nand_3 (nand_3_out, not_2_out, PHI0_out);
  not not_10 (not_10_out, and_5_out);
  nand nand_4 (nand_4_out, not_6_out, PHI0_out);
  not not_11 (not_11_out, and_4_out);
  nand nand_5 (nand_5_out, not_3_out, PHI0_out);
  not not_12 (not_12_out, and_7_out);
  nand nand_6 (nand_6_out, not_7_out, PHI0_out);
  not not_13 (not_13_out, and_6_out);
  D_LATCH d_latch_1 (.EN(PHI0_out), .in(and_1_out), .out(d_latch_1_out));  // open: out_2
  and and_2 (and_2_out, nand_1_out, not_8_out);
  and and_3 (and_3_out, nand_2_out, not_9_out);
  and and_4 (and_4_out, nand_3_out, not_10_out);
  and and_5 (and_5_out, nand_4_out, not_11_out);
  and and_6 (and_6_out, nand_5_out, not_12_out);
  and and_7 (and_7_out, nand_6_out, not_13_out);
  not not_14 (not_14_out, d_latch_1_out);
  not not_15 (not_15_out, and_3_out);
  not not_16 (not_16_out, PHI0_out);
  not not_17 (not_17_out, PHI0_out);
  nand nand_7 (nand_7_out, nready, d_latch_4_out_2);
  and and_8 (and_8_out, nand_7_out, not_14_out);
  D_LATCH d_latch_2 (.EN(not_16_out), .in(and_5_out), .out_2(d_latch_2_out_2));  // open: out
  D_LATCH d_latch_3 (.EN(not_17_out), .in(and_6_out), .out_2(d_latch_3_out_2));  // open: out
  not not_18 (not_18_out, PHI0_out);
  D_LATCH d_latch_4 (.EN(not_18_out), .in(and_8_out), .out_2(d_latch_4_out_2));  // open: out
  D_LATCH d_latch_5 (.EN(PHI0_out), .in(d_latch_4_out_2), .out_2(d_latch_5_out_2));  // open: out
  nor nor_1 (nor_1_out, d_latch_4_out_2, BRK5);
  not not_19 (not_19_out, PHI0_out);
  not not_20 (not_20_out, nready);
  not not_21 (not_21_out, d_latch_5_out_2);
  D_LATCH d_latch_6 (.EN(not_19_out), .in(not_15_out), .out(d_latch_6_out));  // open: out_2
  D_LATCH d_latch_7 (.EN(PHI0_out), .in(nor_1_out), .out_2(d_latch_7_out_2));  // open: out
  and and_9 (and_9_out, not_21_out, not_20_out);
  D_LATCH d_latch_8 (.EN(PHI0_out), .in(nor_6_out), .out_2(d_latch_8_out_2));  // open: out
  D_LATCH d_latch_9 (.EN(PHI0_out), .in(nor_6_out), .out(d_latch_9_out));  // open: out_2
  not not_22 (not_22_out, PHI0_out);
  D_LATCH d_latch_10 (.EN(not_22_out), .in(and_9_out), .out(d_latch_10_out));  // open: out_2
  not not_23 (not_23_out, not_21_out);
  not not_24 (not_24_out, PHI0_out);
  D_LATCH d_latch_11 (.EN(PHI0_out), .in(d_latch_3_out_2), .out(d_latch_11_out));  // open: out_2
  D_LATCH d_latch_12 (.EN(not_25_out), .in(nor_9_out), .out(d_latch_12_out));  // open: out_2
  not not_25 (not_25_out, PHI0_out);
  not not_26 (not_26_out, and_10_out);
  and and_10 (and_10_out, nI_OUT, not_23_out);
  D_LATCH d_latch_13 (.EN(not_27_out), .in(nor_11_out), .out(d_latch_13_out));  // open: out_2
  not not_27 (not_27_out, PHI0_out);
  D_LATCH d_latch_14 (.EN(PHI0_out), .in(nor_4_out), .out(d_latch_14_out));  // open: out_2
  D_LATCH d_latch_15 (.EN(not_24_out), .in(d_latch_8_out_2), .out(d_latch_15_out));  // open: out_2
  nor nor_2 (nor_2_out, d_latch_9_out, d_latch_10_out);
  nor nor_3 (nor_3_out, d_latch_2_out_2, not_26_out);
  not not_28 (not_28_out, nor_6_out);
  not not_29 (not_29_out, d_latch_13_out);
  nor nor_4 (nor_4_out, d_latch_6_out, nor_5_out);
  nor nor_5 (nor_5_out, d_latch_15_out, d_latch_14_out);
  nor nor_6 (nor_6_out, d_latch_17_out, nor_2_out);
  nor nor_7 (nor_7_out, d_latch_11_out, d_latch_12_out);
  or or_1 (or_1_out, nor_3_out, not_28_out);
  D_LATCH d_latch_16 (.EN(PHI0_out), .in(and_11_out), .out(d_latch_16_out));  // open: out_2
  and and_11 (and_11_out, or_2_out, not_29_out);
  nor nor_8 (nor_8_out, d_latch_7_out_2, not_15_out, nor_4_out);
  not not_30 (DORES, nor_7_out);
  nor nor_9 (nor_9_out, nor_7_out, not_21_out);
  nor nor_10 (nor_10_out, BR2, T0);
  not not_31 (not_31_out, or_1_out);
  not not_32 (not_32_out, PHI0_out);
  or or_2 (or_2_out, nor_10_out, not_31_out);
  nor nor_11 (nor_11_out, d_latch_16_out, not_21_out);
  D_LATCH d_latch_17 (.EN(not_32_out), .in(nor_8_out), .out(d_latch_17_out));  // open: out_2
  nor nor_12 (B_OUT, DORES, nor_11_out);
  not not_33 (not_33_out, BRK5);
  or or_3 (or_3_out, nor_1_out, not_34_out);
  not not_34 (not_34_out, DORES);
  nor nor_13 (nor_13_out, nor_1_out, nor_6_out, DORES);
  D_LATCH d_latch_18 (.EN(PHI0_out), .in(not_33_out), .out_2(_0_ADL0));  // open: out
  D_LATCH d_latch_19 (.EN(PHI0_out), .in(or_3_out), .out_2(_0_ADL1));  // open: out
  D_LATCH d_latch_20 (.EN(PHI0_out), .in(nor_13_out), .out_2(d_latch_20_out_2));  // open: out
  not not_35 (_0_ADL2, d_latch_20_out_2);

  // Notes on the sheet:
  //   6502 INTERRUPT HANDLING
  //   INPUT TRIGGERS
  //   INTERRUPT CYCLE 6-7
  //   /NMIP
  //   /IRQP
  //   RESP
  //   /ready
  //   BRK6E
  //   BRK7
  //   BRK6E
  //   BRK7
  //   /I_OUT
  //   BRK6E
  //   NMI EDGE DETECT
  //   /IRQP
  //   /DONMI
  //   B FLAG
  //   RESET FLIP/FLOP
  //   BRK6E
  //   BR2
  //   T0
  //   IRQ CHECK
  //   /DONMI
  //   DORES
  //   BRK5
  //   BRK7
  //   INTERRUPT ADDRESS
endmodule

module D_LATCH (
  input  EN,
  input  in,
  output out,
  output out_2
);

  D_Flip_Flop d_ff_1 (.clk(EN), .D(in), .Q(out), .Qn(out_2));  // open: preset, en, reset
endmodule
