// Logisim project RANDOM.circ as structural Verilog: 12 circuits, main circuit RANDOM
module main (
  input  nNMI,
  input  nIRQ,
  input  nRES,
  input  SO,
  input  RDY,
  input  in_6,
  input  D0_IN,
  input  D1_IN,
  input  D2_IN,
  input  D3_IN,
  input  D4_IN,
  input  D5_IN,
  input  D6_IN,
  input  D7_IN,
  input  in_15,
  input  in_16,
  input  in_17,
  input  in_18,
  input  in_19,
  input  in_20,
  input  in_21
);

  wire decoder_trans_1__0, decoder_trans_1__1, decoder_trans_1__2, decoder_trans_1__3, decoder_trans_1__4,
       decoder_trans_1__5, decoder_trans_1__6, decoder_trans_1__7, decoder_trans_1__8, decoder_trans_1__9,
       decoder_trans_1__10, decoder_trans_1__11, decoder_trans_1__12, decoder_trans_1__13,
       decoder_trans_1__14, decoder_trans_1__15, decoder_trans_1__16, decoder_trans_1__17,
       decoder_trans_1__18, decoder_trans_1__19, decoder_trans_1__20, decoder_trans_1__21,
       decoder_trans_1__22, decoder_trans_1__23, decoder_trans_1__24, decoder_trans_1__25,
       decoder_trans_1__26, decoder_trans_1__27, decoder_trans_1__28, decoder_trans_1__29,
       decoder_trans_1__30, decoder_trans_1__31, decoder_trans_1__32, decoder_trans_1__33,
       decoder_trans_1__34, decoder_trans_1__35, decoder_trans_1__36, decoder_trans_1__37,
       decoder_trans_1__38, decoder_trans_1__39, decoder_trans_1__40, decoder_trans_1__41,
       decoder_trans_1__42, decoder_trans_1__43, decoder_trans_1__44, decoder_trans_1__45,
       decoder_trans_1__46, decoder_trans_1__47, decoder_trans_1__48, decoder_trans_1__49,
       decoder_trans_1__50, decoder_trans_1__51, decoder_trans_1__52, decoder_trans_1__53,
       decoder_trans_1__54, decoder_trans_1__55, decoder_trans_1__56, decoder_trans_1__57,
       decoder_trans_1__58, decoder_trans_1__59, decoder_trans_1__60, decoder_trans_1__61,
       decoder_trans_1__62, decoder_trans_1__63, decoder_trans_1__64, decoder_trans_1__65,
       decoder_trans_1__66, decoder_trans_1__67, decoder_trans_1__68, decoder_trans_1__69,
       decoder_trans_1__70, decoder_trans_1__71, decoder_trans_1__72, decoder_trans_1__73,
       decoder_trans_1__74, decoder_trans_1__75, decoder_trans_1__76, decoder_trans_1__77,
       decoder_trans_1__78, decoder_trans_1__79, decoder_trans_1__80, decoder_trans_1__81,
       decoder_trans_1__82, decoder_trans_1__83, decoder_trans_1__84, decoder_trans_1__85,
       decoder_trans_1__86, decoder_trans_1__87, decoder_trans_1__88, decoder_trans_1__89,
       decoder_trans_1__90, decoder_trans_1__91, decoder_trans_1__92, decoder_trans_1__93,
       decoder_trans_1__94, decoder_trans_1__95, decoder_trans_1__96, decoder_trans_1__97,
       decoder_trans_1__98, decoder_trans_1__99, decoder_trans_1__100, decoder_trans_1__101,
       decoder_trans_1__102, decoder_trans_1__103, decoder_trans_1__104, decoder_trans_1__105,
       decoder_trans_1__106, decoder_trans_1__107, decoder_trans_1__108, decoder_trans_1__109,
       decoder_trans_1__110, decoder_trans_1__111, decoder_trans_1__112, decoder_trans_1__113,
       decoder_trans_1__114, decoder_trans_1__115, decoder_trans_1__116, decoder_trans_1__117,
       decoder_trans_1__118, decoder_trans_1__119, decoder_trans_1__120, decoder_trans_1__121,
       decoder_trans_1__122, decoder_trans_1__123, decoder_trans_1__124, decoder_trans_1__125,
       decoder_trans_1__126, decoder_trans_1__127, decoder_trans_1__128, decoder_trans_1__129, int_1__0_adl0,
       int_1__0_adl1, int_1__0_adl2, int_1_b_out, int_1_brk6e, int_1_dores, int_1_resp, ir_1_ir0, ir_1_ir1,
       ir_1_ir2, ir_1_ir3, ir_1_ir4, ir_1_ir5, ir_1_ir6, ir_1_ir7, not_1_out, not_2_out, not_3_out,
       not_4_out, not_5_out, not_6_out, not_7_out, not_8_out, not_9_out, PHI0_out, predecode_1_nimplied,
       predecode_1_ntwocycle, predecode_1_pd0, predecode_1_pd1, predecode_1_pd2, predecode_1_pd3,
       predecode_1_pd4, predecode_1_pd5, predecode_1_pd6, predecode_1_pd7, random_1__0_add, random_1__0_adh0,
       random_1__0_adh17, random_1__0_ir, random_1__0_v, random_1__1_pc, random_1__1_v, random_1_ac_db,
       random_1_ac_sb, random_1_acr_c, random_1_add_adl, random_1_add_sb06, random_1_add_sb7,
       random_1_adh_abh, random_1_adh_pch, random_1_adl_abl, random_1_adl_add, random_1_adl_pcl,
       random_1_ands, random_1_avr_v, random_1_br2, random_1_brk5, random_1_db_add, random_1_db_c,
       random_1_db_n, random_1_db_p, random_1_db_v, random_1_dbz_z, random_1_dl_adh, random_1_dl_adl,
       random_1_dl_db, random_1_eors, random_1_fetch, random_1_ir5_c, random_1_ir5_d, random_1_ir5_i,
       random_1_nacin, random_1_ndaa, random_1_ndb_add, random_1_ndsa, random_1_nready, random_1_nt0x,
       random_1_nt1x, random_1_nt2, random_1_nt3, random_1_nt4, random_1_nt5, random_1_ors, random_1_p_db,
       random_1_pch_adh, random_1_pch_db, random_1_pch_pch, random_1_pcl_adl, random_1_pcl_db,
       random_1_pcl_pcl, random_1_rd, random_1_rw, random_1_s_adl, random_1_s_s, random_1_s_sb,
       random_1_sb_ac, random_1_sb_add, random_1_sb_adh, random_1_sb_db, random_1_sb_s, random_1_sb_x,
       random_1_sb_y, random_1_srs, random_1_sums, random_1_sync, random_1_t0, random_1_x_sb, random_1_y_sb;

  Clock PHI0 (.out(PHI0_out));
  INT int_1 (
    .PHI0(PHI0_out), .nNMI(nNMI), .nIRQ(nIRQ), .nRES(nRES), .nI_OUT(in_6), .BR2(random_1_br2),
    .T0(random_1_t0), .BRK5(random_1_brk5), .nready(random_1_nready), ._0_ADL0(int_1__0_adl0),
    ._0_ADL1(int_1__0_adl1), ._0_ADL2(int_1__0_adl2), .DORES(int_1_dores), .RESP(int_1_resp),
    .BRK6E(int_1_brk6e), .B_OUT(int_1_b_out));
  PREDECODE predecode_1 (
    .PHI0(PHI0_out), ._0_IR(random_1__0_ir), .D0(D0_IN), .D1(D1_IN), .D2(D2_IN), .D3(D3_IN), .D4(D4_IN),
    .D5(D5_IN), .D6(D6_IN), .D7(D7_IN), .PD0(predecode_1_pd0), .PD1(predecode_1_pd1), .PD2(predecode_1_pd2),
    .PD3(predecode_1_pd3), .PD4(predecode_1_pd4), .PD5(predecode_1_pd5), .PD6(predecode_1_pd6),
    .PD7(predecode_1_pd7), .nIMPLIED(predecode_1_nimplied), .nTWOCYCLE(predecode_1_ntwocycle));
  not not_1 (not_1_out, predecode_1_pd0);
  not not_2 (not_2_out, predecode_1_pd1);
  not not_3 (not_3_out, predecode_1_pd2);
  not not_4 (not_4_out, predecode_1_pd3);
  not not_5 (not_5_out, predecode_1_pd4);
  not not_6 (not_6_out, predecode_1_pd5);
  not not_7 (not_7_out, predecode_1_pd6);
  not not_8 (not_8_out, predecode_1_pd7);
  IR ir_1 (
    .FETCH(random_1_fetch), .PHI0(PHI0_out), .nPD0(not_1_out), .nPD1(not_2_out), .nPD2(not_3_out),
    .nPD3(not_4_out), .nPD4(not_5_out), .nPD5(not_6_out), .nPD6(not_7_out), .nPD7(not_8_out), .IR0(ir_1_ir0),
    .IR2(ir_1_ir2), .IR3(ir_1_ir3), .IR4(ir_1_ir4), .IR5(ir_1_ir5), .IR6(ir_1_ir6), .IR7(ir_1_ir7),
    .IR1(ir_1_ir1));
  DECODER_TRANS decoder_trans_1 (
    .nT5(random_1_nt5), .nT4(random_1_nt4), .nT3(random_1_nt3), .nT2(random_1_nt2), .IR0(ir_1_ir0),
    .IR1(ir_1_ir1), .IR7(ir_1_ir7), .IR4(ir_1_ir4), .IR3(ir_1_ir3), .IR2(ir_1_ir2), .IR6(ir_1_ir6),
    .IR5(ir_1_ir5), .nT0X(random_1_nt0x), .nT1X(random_1_nt1x), ._0(decoder_trans_1__0),
    ._1(decoder_trans_1__1), ._2(decoder_trans_1__2), ._3(decoder_trans_1__3), ._4(decoder_trans_1__4),
    ._5(decoder_trans_1__5), ._6(decoder_trans_1__6), ._7(decoder_trans_1__7), ._8(decoder_trans_1__8),
    ._9(decoder_trans_1__9), ._10(decoder_trans_1__10), ._11(decoder_trans_1__11), ._12(decoder_trans_1__12),
    ._13(decoder_trans_1__13), ._14(decoder_trans_1__14), ._15(decoder_trans_1__15),
    ._16(decoder_trans_1__16), ._17(decoder_trans_1__17), ._18(decoder_trans_1__18),
    ._19(decoder_trans_1__19), ._20(decoder_trans_1__20), ._21(decoder_trans_1__21),
    ._22(decoder_trans_1__22), ._23(decoder_trans_1__23), ._24(decoder_trans_1__24),
    ._25(decoder_trans_1__25), ._26(decoder_trans_1__26), ._27(decoder_trans_1__27),
    ._28(decoder_trans_1__28), ._29(decoder_trans_1__29), ._30(decoder_trans_1__30),
    ._31(decoder_trans_1__31), ._32(decoder_trans_1__32), ._33(decoder_trans_1__33),
    ._34(decoder_trans_1__34), ._35(decoder_trans_1__35), ._36(decoder_trans_1__36),
    ._37(decoder_trans_1__37), ._38(decoder_trans_1__38), ._39(decoder_trans_1__39),
    ._40(decoder_trans_1__40), ._41(decoder_trans_1__41), ._42(decoder_trans_1__42),
    ._43(decoder_trans_1__43), ._44(decoder_trans_1__44), ._45(decoder_trans_1__45),
    ._46(decoder_trans_1__46), ._47(decoder_trans_1__47), ._48(decoder_trans_1__48),
    ._49(decoder_trans_1__49), ._50(decoder_trans_1__50), ._51(decoder_trans_1__51),
    ._52(decoder_trans_1__52), ._53(decoder_trans_1__53), ._54(decoder_trans_1__54),
    ._55(decoder_trans_1__55), ._56(decoder_trans_1__56), ._57(decoder_trans_1__57),
    ._58(decoder_trans_1__58), ._59(decoder_trans_1__59), ._60(decoder_trans_1__60),
    ._61(decoder_trans_1__61), ._62(decoder_trans_1__62), ._63(decoder_trans_1__63),
    ._64(decoder_trans_1__64), ._65(decoder_trans_1__65), ._66(decoder_trans_1__66),
    ._67(decoder_trans_1__67), ._68(decoder_trans_1__68), ._69(decoder_trans_1__69),
    ._70(decoder_trans_1__70), ._71(decoder_trans_1__71), ._72(decoder_trans_1__72),
    ._73(decoder_trans_1__73), ._74(decoder_trans_1__74), ._75(decoder_trans_1__75),
    ._76(decoder_trans_1__76), ._77(decoder_trans_1__77), ._78(decoder_trans_1__78),
    ._79(decoder_trans_1__79), ._80(decoder_trans_1__80), ._81(decoder_trans_1__81),
    ._82(decoder_trans_1__82), ._83(decoder_trans_1__83), ._84(decoder_trans_1__84),
    ._85(decoder_trans_1__85), ._86(decoder_trans_1__86), ._87(decoder_trans_1__87),
    ._88(decoder_trans_1__88), ._89(decoder_trans_1__89), ._90(decoder_trans_1__90),
    ._91(decoder_trans_1__91), ._92(decoder_trans_1__92), ._93(decoder_trans_1__93),
    ._94(decoder_trans_1__94), ._95(decoder_trans_1__95), ._96(decoder_trans_1__96),
    ._97(decoder_trans_1__97), ._98(decoder_trans_1__98), ._99(decoder_trans_1__99),
    ._100(decoder_trans_1__100), ._101(decoder_trans_1__101), ._102(decoder_trans_1__102),
    ._103(decoder_trans_1__103), ._104(decoder_trans_1__104), ._105(decoder_trans_1__105),
    ._106(decoder_trans_1__106), ._107(decoder_trans_1__107), ._108(decoder_trans_1__108),
    ._109(decoder_trans_1__109), ._110(decoder_trans_1__110), ._111(decoder_trans_1__111),
    ._112(decoder_trans_1__112), ._113(decoder_trans_1__113), ._114(decoder_trans_1__114),
    ._115(decoder_trans_1__115), ._116(decoder_trans_1__116), ._117(decoder_trans_1__117),
    ._118(decoder_trans_1__118), ._119(decoder_trans_1__119), ._120(decoder_trans_1__120),
    ._121(decoder_trans_1__121), ._122(decoder_trans_1__122), ._123(decoder_trans_1__123),
    ._124(decoder_trans_1__124), ._125(decoder_trans_1__125), ._126(decoder_trans_1__126),
    ._127(decoder_trans_1__127), ._128(decoder_trans_1__128), ._129(decoder_trans_1__129));
  not not_9 (not_9_out, ir_1_ir5);
  RANDOM random_1 (
    .BRK6E(int_1_brk6e), ._0_ADL0(int_1__0_adl0), .D0(decoder_trans_1__0), .D1(decoder_trans_1__1),
    .D2(decoder_trans_1__2), .D3(decoder_trans_1__3), .D4(decoder_trans_1__4), .D5(decoder_trans_1__5),
    .D6(decoder_trans_1__6), .D7(decoder_trans_1__7), .D8(decoder_trans_1__8), .D9(decoder_trans_1__9),
    .D10(decoder_trans_1__10), .D11(decoder_trans_1__11), .D12(decoder_trans_1__12),
    .D13(decoder_trans_1__13), .D14(decoder_trans_1__14), .D15(decoder_trans_1__15),
    .D16(decoder_trans_1__16), .D17(decoder_trans_1__17), .D18(decoder_trans_1__18),
    .D19(decoder_trans_1__19), .D20(decoder_trans_1__20), .D21(decoder_trans_1__21),
    .D22(decoder_trans_1__22), .D23(decoder_trans_1__23), .D24(decoder_trans_1__24),
    .D25(decoder_trans_1__25), .D26(decoder_trans_1__26), .D27(decoder_trans_1__27),
    .D28(decoder_trans_1__28), .D29(decoder_trans_1__29), .D30(decoder_trans_1__30),
    .D31(decoder_trans_1__31), .D32(decoder_trans_1__32), .D33(decoder_trans_1__33),
    .D34(decoder_trans_1__34), .D35(decoder_trans_1__35), .D36(decoder_trans_1__36),
    .D37(decoder_trans_1__37), .D38(decoder_trans_1__38), .D39(decoder_trans_1__39),
    .D40(decoder_trans_1__40), .D41(decoder_trans_1__41), .D42(decoder_trans_1__42),
    .D43(decoder_trans_1__43), .D44(decoder_trans_1__44), .D45(decoder_trans_1__45),
    .D46(decoder_trans_1__46), .D47(decoder_trans_1__47), .D48(decoder_trans_1__48),
    .D49(decoder_trans_1__49), .D50(decoder_trans_1__50), .D51(decoder_trans_1__51),
    .D52(decoder_trans_1__52), .D53(decoder_trans_1__53), .D54(decoder_trans_1__54),
    .D55(decoder_trans_1__55), .D56(decoder_trans_1__56), .D57(decoder_trans_1__57),
    .D58(decoder_trans_1__58), .D59(decoder_trans_1__59), .D60(decoder_trans_1__60),
    .D61(decoder_trans_1__61), .D62(decoder_trans_1__62), .D63(decoder_trans_1__63),
    .D64(decoder_trans_1__64), .D65(decoder_trans_1__65), .D66(decoder_trans_1__66),
    .D67(decoder_trans_1__67), .D68(decoder_trans_1__68), .D69(decoder_trans_1__69),
    .D70(decoder_trans_1__70), .D71(decoder_trans_1__71), .D72(decoder_trans_1__72),
    .D73(decoder_trans_1__73), .D74(decoder_trans_1__74), .D75(decoder_trans_1__75),
    .D76(decoder_trans_1__76), .D77(decoder_trans_1__77), .D78(decoder_trans_1__78),
    .D79(decoder_trans_1__79), .D80(decoder_trans_1__80), .D81(decoder_trans_1__81),
    .D82(decoder_trans_1__82), .D83(decoder_trans_1__83), .D84(decoder_trans_1__84),
    .D85(decoder_trans_1__85), .D86(decoder_trans_1__86), .D87(decoder_trans_1__87),
    .D88(decoder_trans_1__88), .D89(decoder_trans_1__89), .D90(decoder_trans_1__90),
    .D91(decoder_trans_1__91), .D92(decoder_trans_1__92), .D93(decoder_trans_1__93),
    .D94(decoder_trans_1__94), .D95(decoder_trans_1__95), .D96(decoder_trans_1__96),
    .D97(decoder_trans_1__97), .D98(decoder_trans_1__98), .D99(decoder_trans_1__99),
    .D100(decoder_trans_1__100), .D101(decoder_trans_1__101), .D102(decoder_trans_1__102),
    .D103(decoder_trans_1__103), .D104(decoder_trans_1__104), .D105(decoder_trans_1__105),
    .D106(decoder_trans_1__106), .D107(decoder_trans_1__107), .D108(decoder_trans_1__108),
    .D109(decoder_trans_1__109), .D110(decoder_trans_1__110), .D111(decoder_trans_1__111),
    .D112(decoder_trans_1__112), .D113(decoder_trans_1__113), .D114(decoder_trans_1__114),
    .D115(decoder_trans_1__115), .D116(decoder_trans_1__116), .D117(decoder_trans_1__117),
    .D118(decoder_trans_1__118), .D119(decoder_trans_1__119), .D120(decoder_trans_1__120),
    .D121(decoder_trans_1__121), .D122(decoder_trans_1__122), .D123(decoder_trans_1__123),
    .D124(decoder_trans_1__124), .D125(decoder_trans_1__125), .D126(decoder_trans_1__126),
    .D127(decoder_trans_1__127), .D128(decoder_trans_1__128), .D129(decoder_trans_1__129), .SO(SO),
    .RESP(int_1_resp), .DORES(int_1_dores), .ACR(in_15), .RDY(RDY), .B_OUT(int_1_b_out),
    .nIMPLIED(predecode_1_nimplied), .nTWOCYCLE(predecode_1_ntwocycle), .nC_OUT(in_16), .nV_OUT(in_17),
    .nN_OUT(in_18), .nZ_OUT(in_19), .nD_OUT(in_20), .nIR5(not_9_out), .DB7(in_21), .BRK5(random_1_brk5),
    .BR2(random_1_br2), .nready(random_1_nready), .T0(random_1_t0), .ADH_ABH(random_1_adh_abh),
    .ADL_ABL(random_1_adl_abl), .Y_SB(random_1_y_sb), .X_SB(random_1_x_sb), .SB_Y(random_1_sb_y),
    .SB_X(random_1_sb_x), .S_SB(random_1_s_sb), .S_ADL(random_1_s_adl), .SB_S(random_1_sb_s),
    .S_S(random_1_s_s), .NDB_ADD(random_1_ndb_add), .DB_ADD(random_1_db_add), ._0_ADD(random_1__0_add),
    .SB_ADD(random_1_sb_add), .ADL_ADD(random_1_adl_add), .ANDS(random_1_ands), .EORS(random_1_eors),
    .ORS(random_1_ors), .nACIN(random_1_nacin), .SRS(random_1_srs), .SUMS(random_1_sums),
    .nDAA(random_1_ndaa), .ADD_SB7(random_1_add_sb7), .ADD_SB06(random_1_add_sb06),
    .ADD_ADL(random_1_add_adl), .nDSA(random_1_ndsa), ._0_ADH0(random_1__0_adh0), .SB_DB(random_1_sb_db),
    .SB_AC(random_1_sb_ac), .SB_ADH(random_1_sb_adh), ._0_ADH17(random_1__0_adh17), .AC_SB(random_1_ac_sb),
    .AC_DB(random_1_ac_db), .ADH_PCH(random_1_adh_pch), .PCH_PCH(random_1_pch_pch), .PCH_DB(random_1_pch_db),
    .PCL_DB(random_1_pcl_db), .PCH_ADH(random_1_pch_adh), .PCL_PCL(random_1_pcl_pcl),
    .PCL_ADL(random_1_pcl_adl), .ADL_PCL(random_1_adl_pcl), .DL_ADL(random_1_dl_adl),
    .DL_ADH(random_1_dl_adh), .DL_DB(random_1_dl_db), .P_DB(random_1_p_db), .ACR_C(random_1_acr_c),
    .AVR_V(random_1_avr_v), .DBZ_Z(random_1_dbz_z), .DB_N(random_1_db_n), .DB_P(random_1_db_p),
    .DB_C(random_1_db_c), .DB_V(random_1_db_v), .IR5_C(random_1_ir5_c), .IR5_I(random_1_ir5_i),
    .IR5_D(random_1_ir5_d), ._0_V(random_1__0_v), ._1_V(random_1__1_v), .RW(random_1_rw),
    .SYNC(random_1_sync), ._1_PC(random_1__1_pc), .FETCH(random_1_fetch), ._0_IR(random_1__0_ir),
    .nT0X(random_1_nt0x), .nT1X(random_1_nt1x), .nT2(random_1_nt2), .nT3(random_1_nt3), .nT4(random_1_nt4),
    .nT5(random_1_nt5), .RD(random_1_rd), .PHI0(PHI0_out));  // open: TRESX, T5, T6, ENDS, ENDX, TRES1
endmodule

module RANDOM (
  input  PHI0,
  input  BRK6E,
  input  _0_ADL0,
  input  D0,
  input  D1,
  input  D2,
  input  D3,
  input  D4,
  input  D5,
  input  D6,
  input  D7,
  input  D8,
  input  D9,
  input  D10,
  input  D11,
  input  D12,
  input  D13,
  input  D14,
  input  D15,
  input  D16,
  input  D17,
  input  D18,
  input  D19,
  input  D20,
  input  D21,
  input  D22,
  input  D23,
  input  D24,
  input  D25,
  input  D26,
  input  D27,
  input  D28,
  input  D29,
  input  D30,
  input  D31,
  input  D32,
  input  D33,
  input  D34,
  input  D35,
  input  D36,
  input  D37,
  input  D38,
  input  D39,
  input  D40,
  input  D41,
  input  D42,
  input  D43,
  input  D44,
  input  D45,
  input  D46,
  input  D47,
  input  D48,
  input  D49,
  input  D50,
  input  D51,
  input  D52,
  input  D53,
  input  D54,
  input  D55,
  input  D56,
  input  D57,
  input  D58,
  input  D59,
  input  D60,
  input  D61,
  input  D62,
  input  D63,
  input  D64,
  input  D65,
  input  D66,
  input  D67,
  input  D68,
  input  D69,
  input  D70,
  input  D71,
  input  D72,
  input  D73,
  input  D74,
  input  D75,
  input  D76,
  input  D77,
  input  D78,
  input  D79,
  input  D80,
  input  D81,
  input  D82,
  input  D83,
  input  D84,
  input  D85,
  input  D86,
  input  D87,
  input  D88,
  input  D89,
  input  D90,
  input  D91,
  input  D92,
  input  D93,
  input  D94,
  input  D95,
  input  D96,
  input  D97,
  input  D98,
  input  D99,
  input  D100,
  input  D101,
  input  D102,
  input  D103,
  input  D104,
  input  D105,
  input  D106,
  input  D107,
  input  D108,
  input  D109,
  input  D110,
  input  D111,
  input  D112,
  input  D113,
  input  D114,
  input  D115,
  input  D116,
  input  D117,
  input  D118,
  input  D119,
  input  D120,
  input  D121,
  input  D122,
  input  D123,
  input  D124,
  input  D125,
  input  D126,
  input  D127,
  input  D128,
  input  D129,
  input  SO,
  input  RESP,
  input  DORES,
  input  ACR,
  input  RDY,
  input  B_OUT,
  input  nIMPLIED,
  input  nTWOCYCLE,
  input  nC_OUT,
  input  nV_OUT,
  input  nN_OUT,
  input  nZ_OUT,
  input  nD_OUT,
  input  nIR5,
  input  DB7,
  output BRK5,
  output BR2,
  output nready,
  output T0,
  output ADH_ABH,
  output ADL_ABL,
  output Y_SB,
  output X_SB,
  output SB_Y,
  output SB_X,
  output S_SB,
  output S_ADL,
  output SB_S,
  output S_S,
  output NDB_ADD,
  output DB_ADD,
  output _0_ADD,
  output SB_ADD,
  output ADL_ADD,
  output ANDS,
  output EORS,
  output ORS,
  output nACIN,
  output SRS,
  output SUMS,
  output nDAA,
  output ADD_SB7,
  output ADD_SB06,
  output ADD_ADL,
  output nDSA,
  output _0_ADH0,
  output SB_DB,
  output SB_AC,
  output SB_ADH,
  output _0_ADH17,
  output AC_SB,
  output AC_DB,
  output ADH_PCH,
  output PCH_PCH,
  output PCH_DB,
  output PCL_DB,
  output PCH_ADH,
  output PCL_PCL,
  output PCL_ADL,
  output ADL_PCL,
  output DL_ADL,
  output DL_ADH,
  output DL_DB,
  output P_DB,
  output ACR_C,
  output AVR_V,
  output DBZ_Z,
  output DB_N,
  output DB_P,
  output DB_C,
  output DB_V,
  output IR5_C,
  output IR5_I,
  output IR5_D,
  output _0_V,
  output _1_V,
  output RW,
  output SYNC,
  output _1_PC,
  output FETCH,
  output _0_IR,
  output nT0X,
  output nT1X,
  output nT2,
  output nT3,
  output nT4,
  output nT5,
  output RD,
  output TRES1,
  output TRESX,
  output T5,
  output T6,
  output ENDS,
  output ENDX
);

  wire and_1_out, and_2_out, and_3_out, and_4_out, and_5_out, and_6_out, and_7_out, and_8_out, and_9_out,
       and_10_out, and_11_out, and_12_out, and_13_out, and_14_out, and_15_out, and_16_out, and_17_out,
       and_18_out, and_19_out, and_20_out, and_21_out, and_22_out, and_23_out, and_24_out, and_27_out,
       and_28_out, and_29_out, and_30_out, buffer_5_out, buffer_6_out, buffer_7_out, buffer_8_out,
       buffer_11_out, buffer_12_out, buffer_13_out, buffer_14_out, buffer_15_out, buffer_16_out,
       buffer_17_out, buffer_28_out, buffer_31_out, buffer_32_out, buffer_33_out, buffer_34_out,
       buffer_38_out, buffer_40_out, d_latch_1_out, d_latch_2_out_2, d_latch_3_out, d_latch_4_out,
       d_latch_5_out, d_latch_6_out, d_latch_7_out_2, d_latch_8_out, d_latch_9_out_2, d_latch_10_out,
       d_latch_11_out, d_latch_12_out_2, d_latch_13_out_2, d_latch_14_out, d_latch_15_out, d_latch_16_out_2,
       d_latch_17_out, d_latch_18_out_2, d_latch_19_out, d_latch_20_out, d_latch_21_out, d_latch_22_out,
       d_latch_23_out, d_latch_24_out, d_latch_25_out, d_latch_26_out, d_latch_27_out, d_latch_28_out,
       d_latch_29_out_2, d_latch_30_out, d_latch_31_out_2, d_latch_32_out, d_latch_33_out_2, d_latch_34_out,
       d_latch_35_out_2, d_latch_36_out, d_latch_37_out_2, d_latch_38_out_2, d_latch_39_out_2,
       d_latch_40_out_2, d_latch_41_out, d_latch_42_out, d_latch_43_out, d_latch_44_out_2, d_latch_45_out,
       d_latch_46_out_2, d_latch_47_out_2, d_latch_48_out_2, d_latch_49_out_2, d_latch_50_out,
       d_latch_52_out, d_latch_53_out_2, d_latch_54_out_2, d_latch_55_out_2, d_latch_56_out_2,
       d_latch_57_out_2, d_latch_58_out_2, d_latch_59_out, d_latch_60_out, d_latch_61_out, d_latch_62_out,
       d_latch_63_out_2, d_latch_64_out_2, d_latch_65_out_2, d_latch_66_out_2, d_latch_67_out_2,
       d_latch_68_out_2, d_latch_69_out_2, d_latch_70_out_2, d_latch_71_out_2, d_latch_72_out_2,
       d_latch_73_out_2, d_latch_74_out_2, d_latch_75_out_2, d_latch_76_out_2, d_latch_77_out_2,
       d_latch_78_out_2, d_latch_79_out_2, d_latch_80_out_2, d_latch_81_out_2, d_latch_82_out_2,
       d_latch_83_out_2, d_latch_84_out_2, d_latch_85_out_2, d_latch_86_out_2, d_latch_87_out_2,
       d_latch_90_out_2, d_latch_91_out_2, d_latch_92_out_2, d_latch_93_out_2, d_latch_94_out_2,
       d_latch_95_out_2, d_latch_96_out_2, d_latch_97_out_2, d_latch_98_out_2, d_latch_99_out_2,
       d_latch_100_out_2, d_latch_101_out_2, d_latch_102_out_2, d_latch_103_out_2, d_latch_104_out_2,
       d_latch_105_out_2, d_latch_106_out_2, d_latch_110_out, d_latch_117_out, d_latch_118_out,
       d_latch_119_out, d_latch_120_out, d_latch_121_out, d_latch_122_out, d_latch_123_out, d_latch_124_out,
       d_latch_125_out, d_latch_126_out, multiplexer_1_out, nand_1_out, nand_2_out, nand_3_out, nand_4_out,
       nand_5_out, nand_6_out, nand_7_out, nand_8_out, nand_9_out, nand_10_out, nand_11_out, nand_12_out,
       nand_13_out, nand_14_out, nand_15_out, nand_16_out, nand_17_out, nand_18_out, nand_19_out,
       nand_20_out, nand_21_out, nand_22_out, nand_23_out, nand_24_out, nand_25_out, nand_26_out,
       nand_27_out, nand_28_out, nand_29_out, nand_30_out, nand_31_out, nand_32_out, nand_33_out,
       nand_34_out, nand_35_out, nand_36_out, nand_38_out, nand_39_out, nand_40_out, nand_41_out,
       nand_42_out, nand_43_out, nor_1_out, nor_2_out, nor_3_out, nor_4_out, nor_5_out, nor_6_out, nor_7_out,
       nor_8_out, nor_9_out, nor_10_out, nor_11_out, nor_12_out, nor_13_out, nor_14_out, nor_15_out,
       nor_16_out, nor_17_out, nor_18_out, nor_19_out, nor_20_out, nor_21_out, nor_22_out, nor_23_out,
       nor_24_out, nor_25_out, nor_26_out, nor_27_out, nor_28_out, nor_29_out, nor_30_out, nor_31_out,
       nor_32_out, nor_33_out, nor_34_out, nor_35_out, nor_36_out, nor_37_out, nor_39_out, nor_40_out,
       nor_41_out, nor_42_out, nor_43_out, nor_44_out, nor_45_out, nor_46_out, nor_47_out, nor_48_out,
       nor_49_out, nor_50_out, nor_51_out, nor_52_out, nor_53_out, nor_54_out, nor_55_out, nor_56_out,
       nor_57_out, nor_58_out, nor_59_out, nor_60_out, nor_61_out, nor_62_out, nor_63_out, nor_64_out,
       nor_65_out, nor_66_out, nor_67_out, nor_68_out, nor_69_out, nor_70_out, nor_71_out, nor_72_out,
       nor_74_out, nor_75_out, nor_76_out, nor_77_out, nor_78_out, nor_79_out, nor_80_out, nor_81_out,
       nor_82_out, nor_83_out, nor_84_out, nor_86_out, nor_87_out, nor_88_out, nor_89_out, nor_90_out,
       nor_91_out, nor_92_out, nor_93_out, nor_94_out, nor_95_out, nor_96_out, nor_97_out, nor_98_out,
       nor_99_out, nor_100_out, nor_102_out, nor_103_out, nor_104_out, nor_105_out, nor_106_out, nor_107_out,
       nor_108_out, nor_109_out, nor_110_out, not_1_out, not_2_out, not_3_out, not_4_out, not_5_out,
       not_6_out, not_7_out, not_8_out, not_9_out, not_10_out, not_11_out, not_12_out, not_13_out,
       not_14_out, not_15_out, not_16_out, not_17_out, not_18_out, not_19_out, not_20_out, not_21_out,
       not_22_out, not_23_out, not_24_out, not_25_out, not_26_out, not_27_out, not_28_out, not_29_out,
       not_30_out, not_31_out, not_32_out, not_33_out, not_34_out, not_35_out, not_36_out, not_37_out,
       not_38_out, not_39_out, not_40_out, not_41_out, not_42_out, not_43_out, not_44_out, not_45_out,
       not_46_out, not_47_out, not_48_out, not_49_out, not_50_out, not_51_out, not_52_out, not_53_out,
       not_54_out, not_55_out, not_57_out, not_58_out, not_59_out, not_60_out, not_61_out, not_62_out,
       not_63_out, not_64_out, not_65_out, not_66_out, not_67_out, not_68_out, not_69_out, not_70_out,
       not_71_out, not_72_out, not_73_out, not_74_out, not_75_out, not_76_out, not_77_out, not_78_out,
       not_79_out, not_80_out, not_81_out, not_82_out, not_83_out, not_84_out, not_85_out, not_86_out,
       not_87_out, not_88_out, not_89_out, not_90_out, not_91_out, not_92_out, not_94_out, not_95_out,
       not_96_out, not_99_out, not_100_out, not_101_out, not_102_out, not_103_out, not_104_out, not_105_out,
       not_106_out, not_107_out, not_108_out, not_109_out, not_110_out, not_111_out, not_112_out,
       not_113_out, not_114_out, not_115_out, not_116_out, not_117_out, not_118_out, not_120_out,
       not_121_out, not_122_out, not_123_out, not_124_out, not_125_out, not_126_out, not_127_out,
       not_128_out, not_129_out, not_130_out, not_131_out, not_132_out, not_133_out, not_134_out,
       not_135_out, not_136_out, not_137_out, not_138_out, not_139_out, not_140_out, not_141_out,
       not_142_out, not_143_out, not_144_out, not_145_out, not_146_out, not_147_out, not_148_out,
       not_149_out, or_1_out, or_2_out, or_3_out, or_4_out, or_5_out, or_6_out, or_7_out, or_8_out,
       xnor_1_out;

  not not_1 (not_1_out, d_latch_18_out_2);
  nor nor_1 (nor_1_out, D14, D15, D16);
  not not_2 (not_2_out, D17);
  nor nor_2 (nor_2_out, D18, D19, D20);
  nor nor_3 (nor_3_out, D52, D53);
  nor nor_4 (nor_4_out, D129, D90);
  nor nor_5 (nor_5_out, D100, D101, D102, D103, D104, D105);
  not not_3 (not_3_out, ACR);
  nor nor_6 (nor_6_out, not_1_out, d_latch_2_out_2);
  nor nor_7 (nor_7_out, D1, D2, D3, D4, D5);
  nor nor_8 (nor_8_out, D8, D9, D10, D11, D13);
  not not_4 (not_4_out, D29);
  not not_5 (not_5_out, D93);
  nor nor_9 (nor_9_out, D71, D72);
  not not_6 (not_6_out, D97);
  nor nor_10 (nor_10_out, D111, D122, D123, D124, D125);
  not not_7 (not_7_out, D129);
  not not_8 (not_8_out, DB7);
  D_LATCH d_latch_1 (.EN(PHI0), .in(D80), .out(d_latch_1_out));  // open: out_2
  not not_9 (not_9_out, d_latch_1_out);
  nand nand_1 (nand_1_out, not_3_out, not_1_out);
  not not_10 (not_10_out, nor_6_out);
  D_LATCH d_latch_2 (.EN(PHI0), .in(d_latch_7_out_2), .out_2(d_latch_2_out_2));  // open: out
  not not_11 (not_11_out, D7);
  nand nand_2 (nand_2_out, nor_1_out, nor_2_out);
  nor nor_11 (nor_11_out, D21, D22, D23, D24, D25, D26);
  not not_12 (not_12_out, not_4_out);
  nor nor_12 (nor_12_out, nready, D32);
  not not_13 (not_13_out, nor_12_out);
  not not_14 (not_14_out, D34);
  nor nor_13 (nor_13_out, not_5_out, not_35_out);
  nor nor_14 (nor_14_out, D69, D70);
  not not_15 (not_15_out, nor_14_out);
  not not_16 (not_16_out, D75);
  nand nand_3 (nand_3_out, D76, T5);
  and and_1 (and_1_out, D128, not_7_out);
  D_LATCH d_latch_3 (.EN(not_17_out), .in(TRESX), .out(d_latch_3_out));  // open: out_2
  not not_17 (not_17_out, PHI0);
  D_LATCH d_latch_4 (.EN(not_18_out), .in(nTWOCYCLE), .out(d_latch_4_out));  // open: out_2
  not not_18 (not_18_out, PHI0);
  D_LATCH d_latch_5 (.EN(not_19_out), .in(TRES1), .out(d_latch_5_out));  // open: out_2
  not not_19 (not_19_out, PHI0);
  nand nand_4 (nand_4_out, not_8_out, d_latch_1_out);
  and and_2 (and_2_out, nand_4_out, nand_5_out);
  nand nand_5 (nand_5_out, not_9_out, d_latch_6_out);
  not not_20 (not_20_out, PHI0);
  and and_3 (and_3_out, nand_1_out, not_10_out);
  nand nand_6 (nand_6_out, nor_27_out, D0);
  nand nand_7 (nand_7_out, D6, D7);
  nand nand_8 (nand_8_out, D6, not_11_out);
  nand nand_9 (nand_9_out, nor_27_out, D12);
  not not_21 (not_21_out, PHI0);
  nand nand_10 (nand_10_out, D33, not_14_out);
  nor nor_15 (nor_15_out, D35, D36, D37, D38, D39, nready);
  nor nor_16 (nor_16_out, D39, D40, D41, D42, D43);
  nand nand_11 (nand_11_out, D44, T5);
  nor nor_17 (nor_17_out, D49, D50, nor_13_out);
  not not_22 (not_22_out, nor_17_out);
  nor nor_18 (nor_18_out, T0, T5);
  not not_23 (not_23_out, nor_20_out);
  nor nor_19 (nor_19_out, D58, D59, D60, D61, D62, D63, D64);
  not not_24 (not_24_out, D64);
  not not_25 (not_25_out, RDY);
  not not_26 (not_26_out, and_4_out);
  and and_4 (and_4_out, not_16_out, nand_3_out);
  nor nor_20 (nor_20_out, D81, D82);
  nor nor_21 (nor_21_out, D83, D129);
  nor nor_22 (nor_22_out, D85, D86, D84, D26, D87, D88, D89);
  not not_27 (not_27_out, nor_23_out);
  nor nor_23 (nor_23_out, D89, nor_4_out, D91, D84);
  nor nor_24 (nor_24_out, D94, D95, D96);
  nor nor_25 (nor_25_out, D91, D92);
  nor nor_26 (nor_26_out, D98, D99);
  nor nor_27 (nor_27_out, not_6_out, nor_10_out);
  nor nor_28 (nor_28_out, D106, D107);
  not not_28 (not_28_out, D113);
  nor nor_29 (nor_29_out, D114, D115);
  nand nand_12 (nand_12_out, d_latch_3_out, d_latch_4_out);
  not not_29 (not_29_out, d_latch_5_out);
  not not_30 (not_30_out, PHI0);
  D_LATCH d_latch_6 (.EN(PHI0), .in(d_latch_12_out_2), .out(d_latch_6_out));  // open: out_2
  D_LATCH d_latch_7 (.EN(not_20_out), .in(and_3_out), .out_2(d_latch_7_out_2));  // open: out
  D_LATCH d_latch_8 (.EN(not_21_out), .in(nready), .out(d_latch_8_out));  // open: out_2
  and and_5 (and_5_out, nand_10_out, nor_15_out);
  and and_6 (and_6_out, nor_16_out, nand_11_out);
  nor nor_30 (nor_30_out, nor_18_out, nC_OUT);
  nor nor_31 (nor_31_out, D57, not_23_out);
  nand nand_13 (nand_13_out, D65, not_24_out);
  nor nor_32 (nor_32_out, D66, D67, D68, not_15_out);
  D_LATCH d_latch_9 (.EN(PHI0), .in(not_25_out), .out_2(d_latch_9_out_2));  // open: out
  not not_31 (not_31_out, PHI0);
  D_LATCH d_latch_10 (.EN(PHI0), .in(not_28_out), .out(d_latch_10_out));  // open: out_2
  D_LATCH d_latch_11 (.EN(PHI0), .in(nor_29_out), .out(d_latch_11_out));  // open: out_2
  nor nor_33 (nor_33_out, RDY, d_latch_15_out);
  nor nor_34 (nor_34_out, d_latch_14_out, and_9_out, d_latch_28_out);
  nand nand_14 (nand_14_out, not_6_out, nor_28_out);
  and and_7 (and_7_out, nand_12_out, not_29_out);
  D_LATCH d_latch_12 (.EN(not_30_out), .in(and_2_out), .out_2(d_latch_12_out_2));  // open: out
  not not_32 (not_32_out, and_6_out);
  not not_33 (not_33_out, nor_30_out);
  and and_8 (and_8_out, nand_13_out, nor_32_out);
  D_LATCH d_latch_13 (.EN(not_31_out), .in(d_latch_9_out_2), .out_2(d_latch_13_out_2));  // open: out
  D_LATCH d_latch_14 (.EN(PHI0), .in(nor_33_out), .out(d_latch_14_out));  // open: out_2
  not not_34 (not_34_out, PHI0);
  D_LATCH d_latch_15 (.EN(not_34_out), .in(nor_34_out), .out(d_latch_15_out));  // open: out_2
  and and_9 (and_9_out, nand_14_out, DORES);
  nor nor_35 (nor_35_out, d_latch_19_out, d_latch_20_out);
  not not_35 (not_35_out, d_latch_12_out_2);
  D_LATCH d_latch_16 (.EN(not_36_out), .in(nready), .out_2(d_latch_16_out_2));  // open: out
  not not_36 (not_36_out, PHI0);
  and and_10 (and_10_out, nand_6_out, nor_7_out, nand_7_out);
  and and_11 (and_11_out, nand_8_out, nor_8_out, nand_9_out);
  nand nand_15 (nand_15_out, D0, nor_27_out);
  nand nand_16 (nand_16_out, nor_27_out, D12);
  nand nand_17 (nand_17_out, D21, not_37_out);
  not not_37 (not_37_out, d_latch_8_out);
  not not_38 (not_38_out, D48);
  nor nor_36 (nor_36_out, not_32_out, BRK6E, D48, D45, D46, D47);
  or or_1 (or_1_out, not_33_out, nor_3_out);
  nand nand_18 (nand_18_out, or_1_out, not_39_out);
  not not_39 (not_39_out, D54);
  nor nor_37 (nor_37_out, D112, D116, D117, D118, D119);
  and and_12 (and_12_out, nor_37_out, nand_19_out);
  nand nand_19 (nand_19_out, D107, T6);
  buf buffer_1 (nready, d_latch_14_out);
  nor nor_38 (nT0X, and_7_out, nor_35_out);
  nor nor_39 (nor_39_out, and_7_out, nor_35_out);
  nor nor_40 (nor_40_out, d_latch_19_out, nready);
  not not_40 (not_40_out, D121);
  not not_41 (not_41_out, D126);
  not not_42 (not_42_out, D126);
  not not_43 (not_43_out, D121);
  nor nor_41 (nor_41_out, D80, D93);
  and and_13 (and_13_out, nand_15_out, nand_16_out);
  and and_14 (and_14_out, nand_17_out, not_44_out);
  not not_44 (not_44_out, D35);
  nor nor_42 (nor_42_out, nor_11_out, d_latch_8_out);
  nor nor_43 (nor_43_out, not_38_out, nready);
  nor nor_44 (nor_44_out, D30, D31, D47, nready, nor_42_out, not_32_out, D45, BRK6E, D48);
  not not_45 (not_45_out, D47);
  not not_46 (not_46_out, nor_36_out);
  not not_47 (not_47_out, nor_19_out);
  nor nor_45 (nor_45_out, d_latch_13_out_2, D73);
  not not_48 (not_48_out, nor_9_out);
  nor nor_46 (nor_46_out, D77, D78);
  nor nor_47 (nor_47_out, nor_24_out, d_latch_8_out);
  not not_49 (not_49_out, T0);
  D_LATCH d_latch_17 (.EN(PHI0), .in(D109), .out(d_latch_17_out));  // open: out_2
  not not_50 (not_50_out, PHI0);
  nor nor_48 (nor_48_out, nC_OUT, D126, not_40_out);
  nor nor_49 (nor_49_out, nV_OUT, D121, not_41_out);
  nor nor_50 (nor_50_out, nN_OUT, not_42_out, not_43_out);
  nor nor_51 (nor_51_out, nZ_OUT, D121, D126);
  not not_51 (not_51_out, nor_41_out);
  D_LATCH d_latch_18 (.EN(PHI0), .in(d_latch_16_out_2), .out_2(d_latch_18_out_2));  // open: out
  not not_52 (not_52_out, d_latch_8_out);
  nor nor_52 (nor_52_out, nor_42_out, nor_43_out, D13);
  nor nor_53 (nor_53_out, not_45_out, and_5_out);
  nor nor_54 (nor_54_out, not_47_out, nand_2_out, T6, not_15_out);
  nand nand_20 (nand_20_out, nor_9_out, not_53_out);
  not not_53 (not_53_out, nor_45_out);
  nor nor_55 (nor_55_out, not_48_out, nready);
  nor nor_56 (nor_56_out, T5, T6);
  not not_54 (not_54_out, D74);
  nand nand_21 (nand_21_out, D79, nor_27_out);
  nor nor_57 (nor_57_out, nor_47_out, not_49_out);
  nor nor_58 (nor_58_out, not_49_out, nor_24_out);
  not not_55 (not_55_out, d_latch_8_out);
  nor nor_59 (nor_59_out, nready, ENDX);
  D_LATCH d_latch_19 (.EN(PHI0), .in(nor_39_out), .out(d_latch_19_out));  // open: out_2
  not not_56 (T0, nor_39_out);
  D_LATCH d_latch_20 (.EN(not_50_out), .in(nor_40_out), .out(d_latch_20_out), .out_2(nT1X));
  nor nor_60 (nor_60_out, nor_48_out, nor_49_out, nor_50_out, nor_51_out);
  nand nand_22 (nand_22_out, D80, and_18_out);
  nor nor_61 (nor_61_out, and_17_out, not_51_out);
  not not_57 (not_57_out, nor_61_out);
  not not_58 (not_58_out, D93);
  nor nor_62 (nor_62_out, not_58_out, d_latch_18_out_2);
  nand nand_23 (nand_23_out, not_52_out, and_3_out);
  not not_59 (not_59_out, not_26_out);
  nand nand_24 (nand_24_out, nor_55_out, nor_56_out);
  and and_15 (and_15_out, not_54_out, nand_21_out);
  D_LATCH d_latch_21 (.EN(PHI0), .in(nor_46_out), .out(d_latch_21_out));  // open: out_2
  not not_60 (not_60_out, nor_69_out);
  nor nor_63 (nor_63_out, not_60_out, T0, D84);
  nand nand_25 (nand_25_out, D93, not_55_out);
  D_LATCH d_latch_22 (.EN(PHI0), .in(nor_25_out), .out(d_latch_22_out));  // open: out_2
  nor nor_64 (nor_64_out, RESP, ENDS, nor_59_out);
  nand nand_26 (nand_26_out, nIR5, nor_60_out);
  nor nor_65 (nor_65_out, nIR5, nor_60_out);
  and and_16 (and_16_out, nand_22_out, not_57_out);
  D_LATCH d_latch_23 (.EN(PHI0), .in(nor_62_out), .out(d_latch_23_out));  // open: out_2
  nor nor_66 (nor_66_out, nand_23_out, nor_89_out);
  D_LATCH d_latch_24 (.EN(PHI0), .in(nor_53_out), .out(d_latch_24_out));  // open: out_2
  D_LATCH d_latch_25 (.EN(PHI0), .in(not_32_out), .out(d_latch_25_out));  // open: out_2
  D_LATCH d_latch_26 (.EN(PHI0), .in(not_22_out), .out(d_latch_26_out));  // open: out_2
  D_LATCH d_latch_27 (.EN(PHI0), .in(nand_18_out), .out(d_latch_27_out));  // open: out_2
  not not_61 (not_61_out, nC_OUT);
  nor nor_67 (nor_67_out, d_latch_8_out, not_59_out);
  not not_62 (not_62_out, D48);
  not not_63 (not_63_out, PHI0);
  nor nor_68 (nor_68_out, d_latch_21_out, nready);
  nor nor_69 (nor_69_out, nor_21_out, SYNC, D80, D56, nor_57_out);
  and and_17 (and_17_out, nor_63_out, nand_25_out);
  D_LATCH d_latch_28 (.EN(PHI0), .in(nor_70_out), .out(d_latch_28_out));  // open: out_2
  nor nor_70 (nor_70_out, D100, D98, T5, nor_27_out, T6, nand_30_out);
  nor nor_71 (nor_71_out, nready, d_latch_2_out_2, and_9_out, d_latch_22_out);
  D_LATCH d_latch_29 (.EN(PHI0), .in(nor_64_out), .out_2(d_latch_29_out_2));  // open: out
  not not_64 (not_64_out, nor_65_out);
  D_LATCH d_latch_30 (.EN(PHI0), .in(and_16_out), .out(d_latch_30_out));  // open: out_2
  not not_65 (not_65_out, nIMPLIED);
  D_LATCH d_latch_31 (.EN(PHI0), .in(not_61_out), .out_2(d_latch_31_out_2));  // open: out
  D_LATCH d_latch_32 (.EN(PHI0), .in(nor_67_out), .out(d_latch_32_out));  // open: out_2
  nand nand_27 (nand_27_out, D55, T5);
  nand nand_28 (nand_28_out, not_62_out, and_13_out);
  D_LATCH d_latch_33 (.EN(not_63_out), .in(nor_68_out), .out_2(d_latch_33_out_2));  // open: out
  nor nor_72 (nor_72_out, nor_69_out, nor_45_out, nor_58_out);
  Transistor #(.\type ("n")) transistor_1 (.in(1'b0), .out(SO), .gate(1'b0));
  nor nor_73 (TRESX, nor_71_out, BRK6E, d_latch_29_out_2);
  nor nor_74 (nor_74_out, nor_28_out, nor_10_out, nready);
  and and_18 (and_18_out, nand_26_out, not_64_out);
  xnor xnor_1 (xnor_1_out, not_35_out, ACR);
  and and_19 (and_19_out, xnor_1_out, d_latch_23_out);
  nor nor_75 (nor_75_out, D28, not_96_out, D56, not_27_out);
  nor nor_76 (nor_76_out, d_latch_24_out, d_latch_25_out, d_latch_26_out, d_latch_27_out);
  not not_66 (not_66_out, d_latch_32_out);
  D_LATCH d_latch_34 (.EN(PHI0), .in(d_latch_46_out_2), .out(d_latch_34_out));  // open: out_2
  nand nand_29 (nand_29_out, D52, not_67_out);
  not not_67 (not_67_out, nD_OUT);
  not not_68 (not_68_out, nor_54_out);
  nor nor_77 (nor_77_out, nor_54_out, not_15_out);
  not not_69 (not_69_out, nand_27_out);
  nand nand_30 (nand_30_out, d_latch_33_out_2, nor_46_out);
  nor nor_78 (nor_78_out, nor_72_out, D93);
  not not_70 (not_70_out, SO);
  D_LATCH d_latch_35 (.EN(PHI0), .in(SYNC), .out_2(d_latch_35_out_2));  // open: out
  D_LATCH d_latch_36 (.EN(PHI0), .in(nor_74_out), .out(d_latch_36_out));  // open: out_2
  not not_71 (not_71_out, nready);
  not not_72 (not_72_out, PHI0);
  nor nor_79 (nor_79_out, d_latch_30_out, nready, not_65_out);
  not not_73 (not_73_out, PHI0);
  not not_74 (not_74_out, PHI0);
  nor nor_80 (nor_80_out, nready, nor_75_out);
  D_LATCH d_latch_37 (.EN(PHI0), .in(not_26_out), .out_2(d_latch_37_out_2));  // open: out
  nand nand_31 (nand_31_out, d_latch_32_out, d_latch_31_out_2);
  nand nand_32 (nand_32_out, not_66_out, d_latch_34_out);
  nand nand_33 (nand_33_out, D51, not_75_out);
  not not_75 (not_75_out, nD_OUT);
  nor nor_81 (nor_81_out, D51, nand_29_out);
  nor nor_82 (nor_82_out, nor_77_out, D67, not_69_out, SYNC, D80, nand_28_out);
  nor nor_83 (nor_83_out, nor_21_out, T0);
  nor nor_84 (nor_84_out, nor_83_out, and_1_out);
  not not_76 (not_76_out, PHI0);
  D_LATCH d_latch_38 (.EN(not_76_out), .in(not_70_out), .out_2(d_latch_38_out_2));  // open: out
  nor nor_85 (FETCH, d_latch_35_out_2, nready);
  not not_77 (not_77_out, PHI0);
  D_LATCH d_latch_39 (.EN(not_77_out), .in(nor_34_out), .out_2(d_latch_39_out_2));  // open: out
  not not_78 (not_78_out, PHI0);
  D_LATCH d_latch_40 (.EN(not_78_out), .in(TRESX), .out_2(d_latch_40_out_2));  // open: out
  nand nand_34 (nand_34_out, d_latch_50_out, nready);
  not not_79 (not_79_out, d_latch_36_out);
  nand nand_35 (nand_35_out, T5, not_71_out);
  not not_80 (not_80_out, SYNC);
  nand nand_36 (nand_36_out, and_18_out, D80);
  not not_81 (not_81_out, T0);
  D_LATCH d_latch_41 (.EN(not_72_out), .in(nor_79_out), .out(d_latch_41_out));  // open: out_2
  D_LATCH d_latch_42 (.EN(not_73_out), .in(B_OUT), .out(d_latch_42_out));  // open: out_2
  D_LATCH d_latch_43 (.EN(not_74_out), .in(and_19_out), .out(d_latch_43_out));  // open: out_2
  nor nor_86 (nor_86_out, nor_80_out, nor_66_out);
  not not_82 (not_82_out, not_83_out);
  not not_83 (not_83_out, D93);
  nor nor_87 (nor_87_out, not_22_out, D51, D56);
  not not_84 (not_84_out, nready);
  not not_85 (not_85_out, not_84_out);
  not not_86 (not_86_out, PHI0);
  not not_87 (not_87_out, PHI0);
  and and_20 (and_20_out, nand_31_out, nand_32_out);
  not not_88 (not_88_out, nor_81_out);
  nand nand_37 (_0_IR, B_OUT, FETCH);
  not not_89 (not_89_out, PHI0);
  buf buffer_2 (RW, d_latch_39_out_2);
  not not_90 (not_90_out, PHI0);
  and and_21 (and_21_out, nand_34_out, not_79_out);
  D_LATCH d_latch_44 (.EN(PHI0), .in(nand_35_out), .out_2(d_latch_44_out_2));  // open: out
  and and_22 (and_22_out, nand_36_out, not_81_out);
  or or_2 (or_2_out, nor_86_out, not_82_out);
  or or_3 (or_3_out, nor_87_out, not_85_out);
  nor nor_88 (nor_88_out, not_15_out, not_12_out, not_13_out, not_26_out);
  D_LATCH d_latch_45 (.EN(not_86_out), .in(d_latch_37_out_2), .out(d_latch_45_out));  // open: out_2
  not not_91 (not_91_out, D27);
  D_LATCH d_latch_46 (.EN(not_87_out), .in(and_20_out), .out_2(d_latch_46_out_2));  // open: out
  D_LATCH d_latch_47 (.EN(PHI0), .in(nand_33_out), .out_2(d_latch_47_out_2));  // open: out
  D_LATCH d_latch_48 (.EN(PHI0), .in(not_88_out), .out_2(d_latch_48_out_2));  // open: out
  nor nor_89 (nor_89_out, nand_20_out, D93);
  D_LATCH d_latch_49 (.EN(PHI0), .in(d_latch_38_out_2), .out_2(d_latch_49_out_2));  // open: out
  not not_92 (not_92_out, PHI0);
  not not_93 (RD, nor_90_out);
  nor nor_90 (nor_90_out, not_89_out, d_latch_39_out_2);
  D_LATCH d_latch_50 (.EN(PHI0), .in(T5), .out(d_latch_50_out));  // open: out_2
  D_LATCH d_latch_51 (.EN(not_90_out), .in(and_21_out), .out_2(T5));  // open: out
  not not_94 (not_94_out, PHI0);
  Multiplexer multiplexer_1 (.in0(and_22_out), .in1(not_80_out), .out(multiplexer_1_out), .sel(nready));  // open: en
  or or_4 (or_4_out, d_latch_41_out, d_latch_43_out);
  and and_23 (and_23_out, or_2_out, not_95_out);
  not not_95 (not_95_out, _0_ADL0);
  nor nor_91 (nor_91_out, d_latch_45_out, not_91_out, d_latch_46_out_2);
  nor nor_92 (nor_92_out, T6, nor_42_out, nand_20_out, SYNC, D56);
  nor nor_93 (nor_93_out, D84, nor_21_out, D93, SYNC, D80, T0);
  not not_96 (not_96_out, nor_93_out);
  nor nor_94 (nor_94_out, D102, T5, not_46_out, nor_84_out, D80);
  D_LATCH d_latch_52 (.EN(not_92_out), .in(d_latch_49_out_2), .out(d_latch_52_out));  // open: out_2
  D_LATCH d_latch_53 (.EN(not_94_out), .in(d_latch_44_out_2), .out_2(d_latch_53_out_2));  // open: out
  not not_97 (T6, d_latch_53_out_2);
  and and_24 (and_24_out, d_latch_42_out, or_4_out);
  not not_98 (_1_PC, and_24_out);
  not not_99 (not_99_out, nor_52_out);
  nand nand_38 (nand_38_out, or_3_out, and_5_out);
  not not_100 (not_100_out, nor_44_out);
  D_LATCH d_latch_54 (.EN(PHI0), .in(not_15_out), .out_2(d_latch_54_out_2));  // open: out
  D_LATCH d_latch_55 (.EN(PHI0), .in(not_12_out), .out_2(d_latch_55_out_2));  // open: out
  D_LATCH d_latch_56 (.EN(PHI0), .in(not_13_out), .out_2(d_latch_56_out_2));  // open: out
  D_LATCH d_latch_57 (.EN(PHI0), .in(not_26_out), .out_2(d_latch_57_out_2));  // open: out
  D_LATCH d_latch_58 (.EN(PHI0), .in(nor_88_out), .out_2(d_latch_58_out_2));  // open: out
  nor nor_95 (nor_95_out, nor_91_out, nor_92_out);
  nor nor_96 (nor_96_out, nand_20_out, nor_22_out);
  not not_101 (not_101_out, and_17_out);
  nor nor_97 (nor_97_out, nor_58_out, not_27_out);
  nor nor_98 (nor_98_out, ACR_C, D109, not_68_out);
  not not_102 (not_102_out, D110);
  not not_103 (not_103_out, D108);
  not not_104 (not_104_out, D120);
  not not_105 (not_105_out, D127);
  nor nor_99 (nor_99_out, d_latch_52_out, d_latch_38_out_2);
  D_LATCH d_latch_59 (.EN(PHI0), .in(SYNC), .out(d_latch_59_out));  // open: out_2
  D_LATCH d_latch_60 (.EN(PHI0), .in(multiplexer_1_out), .out(d_latch_60_out));  // open: out_2
  D_LATCH d_latch_61 (.EN(PHI0), .in(RESP), .out(d_latch_61_out));  // open: out_2
  not not_106 (not_106_out, PHI0);
  not not_107 (not_107_out, nready);
  not not_108 (not_108_out, PHI0);
  not not_109 (not_109_out, PHI0);
  not not_110 (not_110_out, PHI0);
  not not_111 (not_111_out, PHI0);
  not not_112 (not_112_out, PHI0);
  not not_113 (not_113_out, PHI0);
  not not_114 (not_114_out, PHI0);
  not not_115 (not_115_out, nor_96_out);
  not not_116 (not_116_out, PHI0);
  not not_117 (not_117_out, nready);
  nor nor_100 (nor_100_out, not_26_out, DB_P);
  nand nand_39 (nand_39_out, d_latch_117_out, nready);
  not not_118 (not_118_out, d_latch_59_out);
  or or_5 (or_5_out, not_118_out, nready);
  nand nand_40 (nand_40_out, d_latch_119_out, nready);
  or or_6 (or_6_out, not_147_out, nready);
  nand nand_41 (nand_41_out, d_latch_121_out, nready);
  or or_7 (or_7_out, not_148_out, nready);
  nand nand_42 (nand_42_out, d_latch_123_out, nready);
  or or_8 (or_8_out, not_149_out, nready);
  nor nor_101 (ENDS, d_latch_60_out, d_latch_61_out);
  D_LATCH d_latch_62 (.EN(not_106_out), .in(not_107_out), .out(d_latch_62_out));  // open: out_2
  D_LATCH d_latch_63 (.EN(PHI0), .in(and_23_out), .out_2(d_latch_63_out_2));  // open: out
  buf buffer_3 (ADH_ABH, d_latch_63_out_2);
  D_LATCH d_latch_64 (.EN(PHI0), .in(nand_24_out), .out_2(d_latch_64_out_2));  // open: out
  buf buffer_4 (ADL_ABL, d_latch_64_out_2);
  D_LATCH d_latch_65 (.EN(PHI0), .in(and_10_out), .out_2(d_latch_65_out_2));  // open: out
  buf buffer_5 (buffer_5_out, d_latch_65_out_2);
  D_LATCH d_latch_66 (.EN(PHI0), .in(and_11_out), .out_2(d_latch_66_out_2));  // open: out
  buf buffer_6 (buffer_6_out, d_latch_66_out_2);
  D_LATCH d_latch_67 (.EN(PHI0), .in(nor_2_out), .out_2(d_latch_67_out_2));  // open: out
  buf buffer_7 (buffer_7_out, d_latch_67_out_2);
  D_LATCH d_latch_68 (.EN(PHI0), .in(nor_1_out), .out_2(d_latch_68_out_2));  // open: out
  buf buffer_8 (buffer_8_out, d_latch_68_out_2);
  D_LATCH d_latch_69 (.EN(PHI0), .in(not_2_out), .out_2(d_latch_69_out_2));  // open: out
  buf buffer_9 (S_SB, d_latch_69_out_2);
  D_LATCH d_latch_70 (.EN(PHI0), .in(and_14_out), .out_2(d_latch_70_out_2));  // open: out
  buf buffer_10 (S_ADL, d_latch_70_out_2);
  D_LATCH d_latch_71 (.EN(PHI0), .in(nor_52_out), .out_2(d_latch_71_out_2));  // open: out
  buf buffer_11 (buffer_11_out, d_latch_71_out_2);
  D_LATCH d_latch_72 (.EN(PHI0), .in(not_99_out), .out_2(d_latch_72_out_2));  // open: out
  buf buffer_12 (buffer_12_out, d_latch_72_out_2);
  D_LATCH d_latch_73 (.EN(PHI0), .in(or_3_out), .out_2(d_latch_73_out_2));  // open: out
  buf buffer_13 (buffer_13_out, d_latch_73_out_2);
  D_LATCH d_latch_74 (.EN(PHI0), .in(nand_38_out), .out_2(d_latch_74_out_2));  // open: out
  buf buffer_14 (buffer_14_out, d_latch_74_out_2);
  D_LATCH d_latch_75 (.EN(PHI0), .in(nor_44_out), .out_2(d_latch_75_out_2));  // open: out
  buf buffer_15 (buffer_15_out, d_latch_75_out_2);
  D_LATCH d_latch_76 (.EN(PHI0), .in(not_100_out), .out_2(d_latch_76_out_2));  // open: out
  buf buffer_16 (buffer_16_out, d_latch_76_out_2);
  D_LATCH d_latch_77 (.EN(PHI0), .in(and_5_out), .out_2(d_latch_77_out_2));  // open: out
  buf buffer_17 (buffer_17_out, d_latch_77_out_2);
  D_LATCH d_latch_78 (.EN(not_108_out), .in(d_latch_54_out_2), .out_2(d_latch_78_out_2));  // open: out
  buf buffer_18 (ANDS, d_latch_78_out_2);
  D_LATCH d_latch_79 (.EN(not_109_out), .in(d_latch_55_out_2), .out_2(d_latch_79_out_2));  // open: out
  buf buffer_19 (EORS, d_latch_79_out_2);
  D_LATCH d_latch_80 (.EN(not_110_out), .in(d_latch_56_out_2), .out_2(d_latch_80_out_2));  // open: out
  buf buffer_20 (ORS, d_latch_80_out_2);
  D_LATCH d_latch_81 (.EN(not_111_out), .in(nor_76_out), .out_2(d_latch_81_out_2));  // open: out
  not not_119 (nACIN, d_latch_81_out_2);
  D_LATCH d_latch_82 (.EN(not_112_out), .in(d_latch_57_out_2), .out_2(d_latch_82_out_2));  // open: out
  buf buffer_21 (SRS, d_latch_82_out_2);
  D_LATCH d_latch_83 (.EN(not_113_out), .in(d_latch_58_out_2), .out_2(d_latch_83_out_2));  // open: out
  buf buffer_22 (SUMS, d_latch_83_out_2);
  D_LATCH d_latch_84 (.EN(not_114_out), .in(d_latch_47_out_2), .out_2(d_latch_84_out_2));  // open: out
  buf buffer_23 (nDAA, d_latch_84_out_2);
  D_LATCH d_latch_85 (.EN(PHI0), .in(nor_95_out), .out_2(d_latch_85_out_2));  // open: out
  buf buffer_24 (ADD_SB7, d_latch_85_out_2);
  D_LATCH d_latch_86 (.EN(PHI0), .in(nor_92_out), .out_2(d_latch_86_out_2));  // open: out
  buf buffer_25 (ADD_SB06, d_latch_86_out_2);
  D_LATCH d_latch_87 (.EN(PHI0), .in(not_115_out), .out_2(d_latch_87_out_2));  // open: out
  buf buffer_26 (ADD_ADL, d_latch_87_out_2);
  D_LATCH d_latch_88 (.EN(not_116_out), .in(d_latch_48_out_2), .out_2(nDSA));  // open: out
  D_LATCH d_latch_89 (.EN(PHI0), .in(nor_20_out), .out_2(_0_ADH0));  // open: out
  D_LATCH d_latch_90 (.EN(PHI0), .in(nor_82_out), .out_2(d_latch_90_out_2));  // open: out
  buf buffer_27 (SB_DB, d_latch_90_out_2);
  D_LATCH d_latch_91 (.EN(PHI0), .in(nor_19_out), .out_2(d_latch_91_out_2));  // open: out
  buf buffer_28 (buffer_28_out, d_latch_91_out_2);
  D_LATCH d_latch_92 (.EN(PHI0), .in(nor_89_out), .out_2(d_latch_92_out_2));  // open: out
  buf buffer_29 (SB_ADH, d_latch_92_out_2);
  D_LATCH d_latch_93 (.EN(PHI0), .in(nor_31_out), .out_2(d_latch_93_out_2));  // open: out
  buf buffer_30 (_0_ADH17, d_latch_93_out_2);
  D_LATCH d_latch_94 (.EN(PHI0), .in(and_8_out), .out_2(d_latch_94_out_2));  // open: out
  buf buffer_31 (buffer_31_out, d_latch_94_out_2);
  D_LATCH d_latch_95 (.EN(PHI0), .in(and_15_out), .out_2(d_latch_95_out_2));  // open: out
  buf buffer_32 (buffer_32_out, d_latch_95_out_2);
  D_LATCH d_latch_96 (.EN(PHI0), .in(nor_93_out), .out_2(d_latch_96_out_2));  // open: out
  buf buffer_33 (buffer_33_out, d_latch_96_out_2);
  D_LATCH d_latch_97 (.EN(PHI0), .in(not_96_out), .out_2(d_latch_97_out_2));  // open: out
  buf buffer_34 (buffer_34_out, d_latch_97_out_2);
  D_LATCH d_latch_98 (.EN(PHI0), .in(nor_46_out), .out_2(d_latch_98_out_2));  // open: out
  buf buffer_35 (PCH_DB, d_latch_98_out_2);
  D_LATCH d_latch_99 (.EN(PHI0), .in(d_latch_33_out_2), .out_2(d_latch_99_out_2));  // open: out
  buf buffer_36 (PCL_DB, d_latch_99_out_2);
  D_LATCH d_latch_100 (.EN(PHI0), .in(nor_78_out), .out_2(d_latch_100_out_2));  // open: out
  buf buffer_37 (PCH_ADH, d_latch_100_out_2);
  D_LATCH d_latch_101 (.EN(PHI0), .in(not_101_out), .out_2(d_latch_101_out_2));  // open: out
  buf buffer_38 (buffer_38_out, d_latch_101_out_2);
  D_LATCH d_latch_102 (.EN(PHI0), .in(nor_69_out), .out_2(d_latch_102_out_2));  // open: out
  buf buffer_39 (PCL_ADL, d_latch_102_out_2);
  D_LATCH d_latch_103 (.EN(PHI0), .in(and_17_out), .out_2(d_latch_103_out_2));  // open: out
  buf buffer_40 (buffer_40_out, d_latch_103_out_2);
  D_LATCH d_latch_104 (.EN(PHI0), .in(nor_20_out), .out_2(d_latch_104_out_2));  // open: out
  buf buffer_41 (DL_ADL, d_latch_104_out_2);
  D_LATCH d_latch_105 (.EN(PHI0), .in(nor_97_out), .out_2(d_latch_105_out_2));  // open: out
  buf buffer_42 (DL_ADH, d_latch_105_out_2);
  D_LATCH d_latch_106 (.EN(PHI0), .in(nor_94_out), .out_2(d_latch_106_out_2));  // open: out
  buf buffer_43 (DL_DB, d_latch_106_out_2);
  D_LATCH d_latch_107 (.EN(PHI0), .in(nor_26_out), .out_2(P_DB));  // open: out
  D_LATCH d_latch_108 (.EN(PHI0), .in(and_12_out), .out_2(ACR_C));  // open: out
  D_LATCH d_latch_109 (.EN(PHI0), .in(D112), .out(AVR_V));  // open: out_2
  D_LATCH d_latch_110 (.EN(PHI0), .in(nor_98_out), .out(d_latch_110_out), .out_2(DBZ_Z));
  nand nand_43 (nand_43_out, d_latch_11_out, d_latch_110_out);
  and and_25 (DB_N, nand_43_out, not_120_out);
  not not_120 (not_120_out, d_latch_17_out);
  and and_26 (DB_P, d_latch_11_out, not_117_out);
  D_LATCH d_latch_111 (.EN(PHI0), .in(nor_100_out), .out_2(DB_C));  // open: out
  nand nand_44 (DB_V, d_latch_10_out, d_latch_11_out);
  D_LATCH d_latch_112 (.EN(PHI0), .in(not_102_out), .out_2(IR5_C));  // open: out
  D_LATCH d_latch_113 (.EN(PHI0), .in(not_103_out), .out_2(IR5_I));  // open: out
  D_LATCH d_latch_114 (.EN(PHI0), .in(not_104_out), .out_2(IR5_D));  // open: out
  D_LATCH d_latch_115 (.EN(PHI0), .in(not_105_out), .out_2(_0_V));  // open: out
  D_LATCH d_latch_116 (.EN(PHI0), .in(nor_99_out), .out(_1_V));  // open: out_2
  nor nor_102 (nor_102_out, d_latch_40_out_2, d_latch_118_out);
  and and_27 (and_27_out, nand_39_out, or_5_out);
  nor nor_103 (nor_103_out, d_latch_40_out_2, d_latch_120_out);
  and and_28 (and_28_out, nand_40_out, or_6_out);
  nor nor_104 (nor_104_out, d_latch_40_out_2, d_latch_122_out);
  and and_29 (and_29_out, nand_41_out, or_7_out);
  nor nor_105 (nor_105_out, d_latch_40_out_2, d_latch_124_out);
  and and_30 (and_30_out, nand_42_out, or_8_out);
  not not_121 (not_121_out, nor_28_out);
  nor nor_106 (nor_106_out, RESP, d_latch_62_out, d_latch_126_out);
  nor nor_107 (nor_107_out, d_latch_125_out, and_19_out);
  nor nor_108 (nor_108_out, nready, nor_107_out);
  not not_122 (not_122_out, PHI0);
  and and_31 (Y_SB, not_122_out, buffer_5_out);
  not not_123 (not_123_out, PHI0);
  and and_32 (X_SB, not_123_out, buffer_6_out);
  not not_124 (not_124_out, PHI0);
  and and_33 (SB_Y, not_124_out, buffer_7_out);
  not not_125 (not_125_out, PHI0);
  and and_34 (SB_X, not_125_out, buffer_8_out);
  not not_126 (not_126_out, PHI0);
  and and_35 (SB_S, not_126_out, buffer_11_out);
  not not_127 (not_127_out, PHI0);
  and and_36 (S_S, not_127_out, buffer_12_out);
  not not_128 (not_128_out, PHI0);
  and and_37 (NDB_ADD, not_128_out, buffer_13_out);
  not not_129 (not_129_out, PHI0);
  and and_38 (DB_ADD, not_129_out, buffer_14_out);
  not not_130 (not_130_out, PHI0);
  and and_39 (_0_ADD, not_130_out, buffer_15_out);
  not not_131 (not_131_out, PHI0);
  and and_40 (SB_ADD, not_131_out, buffer_16_out);
  not not_132 (not_132_out, PHI0);
  and and_41 (ADL_ADD, not_132_out, buffer_17_out);
  not not_133 (not_133_out, PHI0);
  and and_42 (SB_AC, not_133_out, buffer_28_out);
  not not_134 (not_134_out, PHI0);
  and and_43 (AC_SB, not_134_out, buffer_31_out);
  not not_135 (not_135_out, PHI0);
  and and_44 (AC_DB, not_135_out, buffer_32_out);
  not not_136 (not_136_out, PHI0);
  and and_45 (ADH_PCH, not_136_out, buffer_33_out);
  not not_137 (not_137_out, PHI0);
  and and_46 (PCH_PCH, not_137_out, buffer_34_out);
  not not_138 (not_138_out, PHI0);
  and and_47 (PCL_PCL, not_138_out, buffer_38_out);
  not not_139 (not_139_out, PHI0);
  and and_48 (ADL_PCL, not_139_out, buffer_40_out);
  not not_140 (not_140_out, PHI0);
  not not_141 (not_141_out, PHI0);
  not not_142 (not_142_out, PHI0);
  not not_143 (not_143_out, PHI0);
  not not_144 (not_144_out, nor_5_out);
  nor nor_109 (nor_109_out, nor_10_out, D96, not_121_out);
  not not_145 (not_145_out, PHI0);
  not not_146 (not_146_out, PHI0);
  nor nor_110 (nor_110_out, ENDS, nor_108_out);
  D_LATCH d_latch_117 (.EN(PHI0), .in(nor_102_out), .out(d_latch_117_out));  // open: out_2
  not not_147 (not_147_out, d_latch_117_out);
  D_LATCH d_latch_118 (.EN(not_140_out), .in(and_27_out), .out(d_latch_118_out));  // open: out_2
  D_LATCH d_latch_119 (.EN(PHI0), .in(nor_103_out), .out(d_latch_119_out));  // open: out_2
  not not_148 (not_148_out, d_latch_119_out);
  D_LATCH d_latch_120 (.EN(not_141_out), .in(and_28_out), .out(d_latch_120_out));  // open: out_2
  D_LATCH d_latch_121 (.EN(PHI0), .in(nor_104_out), .out(d_latch_121_out));  // open: out_2
  not not_149 (not_149_out, d_latch_121_out);
  D_LATCH d_latch_122 (.EN(not_142_out), .in(and_29_out), .out(d_latch_122_out));  // open: out_2
  D_LATCH d_latch_123 (.EN(PHI0), .in(nor_105_out), .out(d_latch_123_out));  // open: out_2
  D_LATCH d_latch_124 (.EN(not_143_out), .in(and_30_out), .out(d_latch_124_out));  // open: out_2
  nor nor_111 (ENDX, not_144_out, T6, D93, nor_109_out);
  D_LATCH d_latch_125 (.EN(PHI0), .in(nor_106_out), .out(d_latch_125_out));  // open: out_2
  D_LATCH d_latch_126 (.EN(not_145_out), .in(nor_107_out), .out(d_latch_126_out));  // open: out_2
  D_LATCH d_latch_127 (.EN(not_146_out), .in(nor_110_out), .out_2(SYNC));  // open: out
  not not_150 (TRES1, nor_110_out);
  not not_151 (nT2, nor_102_out);
  not not_152 (nT3, nor_103_out);
  not not_153 (nT4, nor_104_out);
  not not_154 (nT5, nor_105_out);

  assign BR2 = D80;
  assign BRK5 = D22;

  // Notes on the sheet:
  //   Flags
  //   From interrupt control
  //   ACR
  //   #S/SB
  //   RTI/5
  //   T2
  //   STK2
  //   JSR2
  //   SBC0
  //   BR3
  //   JSR/5
  //   RTS/5
  //   RTI/5
  //   BR3
  //   Push/pull
  //   DB7
  //   BR2
  //   #SB/X
  //   #SB/Y
  //   /ready
  //   RET
  //   BRFW
  //   T5
  //   STA
  //   BR2
  //   CSI
  //   BIT1
  //   BIT0
  //   TRESX
  //   /TWOCYCLE
  //   TRES1
  //   STOR
  //   STOR
  //   SBXY
  //   /ready
  //   EORS
  //   /ready
  //   T5
  //   T0
  //   T5
  //   /C_OUT
  //   RDY
  //   Push/pull
  //   RTS/5
  //   JMP/4
  //   AVR/V
  //   CSD
  //   /IR6
  //   /MemOP
  //   /IR7
  //   CLV
  //   IMPL
  //   BRK5
  //   NotReadyPhi1
  //   ORS
  //   #DL/ADL
  //   #SB/AC
  //   #DL/ADL
  //   ABS/2
  //   NOADL
  //   /POUT
  //   STOR
  //   /STORE
  //   /SHIFT
  //   /PIN
  //   RDY
  //   /STORE
  //   /SHIFT
  //   TXS
  //   /ready
  //   BRK6E
  //   JSR2
  //   BRK6E
  //   JSR2
  //   ANDS
  //   Ready delay
  //   SRS
  //   IND
  //   JB
  //   T6
  //   DORES
  //   /ready
  //   ACRL2
  //   ACRL1
  //   /ready
  //   STOR
  //   STOR
  //   JSR2
  //   #ADL/ADD
  //   #0/ADH17
  //   #AC/SB
  //   REST
  //   BRFW
  //   #Y/SB
  //   #X/SB
  //   STK2
  //   RET
  //   INC_SB
  //   JB
  //   NotReadyPhi1
  //   T0
  //   WR
  //   BR2
  //   BR3
  //   STXY
  //   STKOP
  //   SB/ADD
  //   to DL/DB
  //   CSET
  //   SBXY
  //   T6
  //   ANDS
  //   /ready
  //   T5
  //   T6
  //   STA
  //   STOR
  //   #PCH/DB
  //   JB
  //   /ARIT
  //   /ready
  //   /ready
  //   ENDX
  //   /IR5
  //   BR2
  //   /BRTAKEN
  //   #ADL/PCL
  //   BR3
  //   NotReadyPhi1
  //   ACRL2
  //   #S/ADL
  //   #SB/S
  //   CSET
  //   PGX
  //   BR0
  //   BR2
  //   DL/PCH
  //   T0
  //   RTS/5
  //   BR3
  //   NotReadyPhi1
  //   STOR
  //   T6
  //   PC/DB
  //   /ready
  //   ACRL1
  //   91/92
  //   RESP
  //   ENDS
  //   T0
  //   #SB/ADH
  //   /C_OUT
  //   NotReadyPhi1
  //   SRS
  //   /ready
  //   ABS/2
  //   JSR/5
  //   T1
  //   T5
  //   REST
  //   /T0X
  //   /T1X
  //   /IMPLIED
  //   BRFW
  //   ACR
  //   T5
  //   #ADL/ABL
  //   JSR2
  //   STXY
  //   #AC/DB
  //   #PCL/ADL
  //   BR0
  //   BRK6E
  //   /SHIFT
  //   /MemOP
  //   /ready
  //   /ready
  //   T2
  //   #PCH/PCH
  //   JSR/5
  //   IND
  //   /D_OUT
  //   ANDS
  //   BR2
  //   JSXY
  //   #PCL/DB
  //   BR3
  //   #ADL/PCL
  //   SO
  //   T1
  //   /BRTAKEN
  //   SBC0
  //   /ACIN
  //   SRS
  //   SBC0
  //   /D_OUT
  //   SBC0
  //   ZTST
  //   T1
  //   PC/DB
  //   ABS/2
  //   T0
  //   IMPL
  //   B_OUT
  //   /ready
  //   TRESX
  //   /ready
  //   /ready
  //   T1
  //   /ready
  //   /BRTAKEN
  //   BR2
  //   T0
  //   /ready
  //   B_OUT
  //   /ready
  //   BR3
  //   JSR/5
  //   /ready
  //   #ADL/ABL
  //   STKOP
  //   PGX
  //   #PCH/ADH
  //   c
  //   a
  //   b
  //   ROR
  //   T6
  //   T1
  //   #SB/DB
  //   T1
  //   T0
  //   BR2
  //   PGX
  //   BR3
  //   T5
  //   ZTST
  //   0/IR
  //   FETCH
  //   TRES2
  //   0/ADL0
  //   #NDB/ADD
  //   #ADL/ABL
  //   JSR/5
  //   #SB/ADH
  //   JMP/4
  //   BR2
  //   R/W
  //   RESP
  //   #ADL/ADD
  //   #ADD/SB7
  //   #ADD/SB06
  //   PGX
  //   NOADL
  //   #ADD/SB06
  //   #ADH/PCH
  //   DL/PCH
  //   IND
  //   #DL/DB
  //   T1
  //   T5
  //   T6
  //   /ACIN
  //   #PCH/PCH
  //   /ready
  //   SRS
  //   TRES2
  //   /ready
  //   /ready
  //   1/PC
  //   PHI0
  //   ENDS
  //   ENDS
  //   /ready
  //   TRES2
  //   TRES2
  //   TRES2
  //   /MemOP
  //   /SHIFT
  //   RESP
  //   To interrupt control
  //   T6
  //   BR3
  //   ENDX
  //   T1
  //   TRES1
  //   /T2
  //   /T3
  //   /T4
  //   /T5
endmodule

module INT (
  input  PHI0,
  input  nNMI,
  input  nIRQ,
  input  nRES,
  input  nI_OUT,
  input  BR2,
  input  T0,
  input  BRK5,
  input  nready,
  output _0_ADL0,
  output _0_ADL1,
  output _0_ADL2,
  output DORES,
  output RESP,
  output BRK6E,
  output B_OUT
);

  wire ADL2_Latch_out_2, and_1_out, and_2_out, and_3_out, and_4_out, and_5_out, and_6_out, and_7_out,
       and_8_out, and_9_out, and_10_out, and_11_out, BLatch1_out, BLatch2_out, IRQP_Latch_out_2,
       LastLatch_out, Latch1_out, Latch2_out_2, Latch3_out_2, Latch4_out, Latch5_out, Latch6_out,
       Latch7_out_2, Latch8_out, Latch9_out, Latch10_out_2, Latch11_out, Latch12_out, nand_1_out, nand_2_out,
       nand_3_out, nand_4_out, nand_5_out, nand_6_out, nand_7_out, nor_1_out, nor_2_out, nor_3_out,
       nor_4_out, nor_5_out, nor_6_out, nor_7_out, nor_8_out, nor_9_out, nor_10_out, nor_11_out, nor_13_out,
       not_1_out, not_2_out, not_3_out, not_4_out, not_5_out, not_6_out, not_7_out, not_8_out, not_9_out,
       not_10_out, not_11_out, not_12_out, not_13_out, not_14_out, not_15_out, not_16_out, not_17_out,
       not_18_out, not_19_out, not_20_out, not_22_out, not_23_out, not_24_out, not_25_out, not_26_out,
       not_27_out, not_28_out, not_29_out, not_31_out, not_32_out, not_33_out, not_34_out, or_1_out,
       or_2_out, or_3_out;

  Transistor #(.\type ("n")) transistor_1 (.in(1'b0), .out(nRES), .gate(1'b0));
  Transistor #(.\type ("n")) transistor_2 (.in(1'b0), .out(nIRQ), .gate(1'b0));
  Transistor #(.\type ("n")) transistor_3 (.in(1'b0), .out(nNMI), .gate(1'b0));
  not not_1 (not_1_out, nNMI);
  not not_2 (not_2_out, nIRQ);
  not not_3 (not_3_out, nRES);
  not not_4 (not_4_out, nready);
  not not_5 (not_5_out, not_1_out);
  not not_6 (not_6_out, not_2_out);
  not not_7 (not_7_out, not_3_out);
  and and_1 (and_1_out, BRK5, not_4_out);
  nand nand_1 (nand_1_out, not_1_out, PHI0);
  not not_8 (not_8_out, and_3_out);
  nand nand_2 (nand_2_out, not_5_out, PHI0);
  not not_9 (not_9_out, and_2_out);
  nand nand_3 (nand_3_out, not_2_out, PHI0);
  not not_10 (not_10_out, and_5_out);
  nand nand_4 (nand_4_out, not_6_out, PHI0);
  not not_11 (not_11_out, and_4_out);
  nand nand_5 (nand_5_out, not_3_out, PHI0);
  not not_12 (not_12_out, and_7_out);
  nand nand_6 (nand_6_out, not_7_out, PHI0);
  not not_13 (not_13_out, and_6_out);
  D_LATCH Latch1 (.EN(PHI0), .in(and_1_out), .out(Latch1_out));  // open: out_2
  and and_2 (and_2_out, nand_1_out, not_8_out);
  and and_3 (and_3_out, nand_2_out, not_9_out);
  and and_4 (and_4_out, nand_3_out, not_10_out);
  and and_5 (and_5_out, nand_4_out, not_11_out);
  and and_6 (and_6_out, nand_5_out, not_12_out);
  and and_7 (and_7_out, nand_6_out, not_13_out);
  not not_14 (not_14_out, Latch1_out);
  not not_15 (not_15_out, and_3_out);
  not not_16 (not_16_out, PHI0);
  not not_17 (not_17_out, PHI0);
  nand nand_7 (nand_7_out, nready, Latch2_out_2);
  and and_8 (and_8_out, nand_7_out, not_14_out);
  D_LATCH IRQP_Latch (.EN(not_16_out), .in(and_5_out), .out_2(IRQP_Latch_out_2));  // open: out
  D_LATCH RESP_Latch (.EN(not_17_out), .in(and_6_out), .out_2(RESP));  // open: out
  not not_18 (not_18_out, PHI0);
  D_LATCH Latch2 (.EN(not_18_out), .in(and_8_out), .out_2(Latch2_out_2));  // open: out
  D_LATCH Latch3 (.EN(PHI0), .in(Latch2_out_2), .out_2(Latch3_out_2));  // open: out
  nor nor_1 (nor_1_out, Latch2_out_2, BRK5);
  not not_19 (not_19_out, PHI0);
  not not_20 (not_20_out, nready);
  not not_21 (BRK6E, Latch3_out_2);
  D_LATCH Latch6 (.EN(not_19_out), .in(not_15_out), .out(Latch6_out));  // open: out_2
  D_LATCH Latch7 (.EN(PHI0), .in(nor_1_out), .out_2(Latch7_out_2));  // open: out
  and and_9 (and_9_out, BRK6E, not_20_out);
  D_LATCH Latch10 (.EN(PHI0), .in(nor_6_out), .out_2(Latch10_out_2));  // open: out
  D_LATCH Latch8 (.EN(PHI0), .in(nor_6_out), .out(Latch8_out));  // open: out_2
  D_LATCH Latch9 (.EN(not_22_out), .in(and_9_out), .out(Latch9_out));  // open: out_2
  not not_22 (not_22_out, PHI0);
  not not_23 (not_23_out, BRK6E);
  not not_24 (not_24_out, PHI0);
  D_LATCH Latch4 (.EN(PHI0), .in(RESP), .out(Latch4_out));  // open: out_2
  D_LATCH Latch5 (.EN(not_25_out), .in(nor_9_out), .out(Latch5_out));  // open: out_2
  not not_25 (not_25_out, PHI0);
  and and_10 (and_10_out, nI_OUT, not_23_out);
  not not_26 (not_26_out, and_10_out);
  not not_27 (not_27_out, PHI0);
  D_LATCH BLatch1 (.EN(not_27_out), .in(nor_11_out), .out(BLatch1_out));  // open: out_2
  D_LATCH Latch12 (.EN(PHI0), .in(nor_4_out), .out(Latch12_out));  // open: out_2
  D_LATCH Latch11 (.EN(not_24_out), .in(Latch10_out_2), .out(Latch11_out));  // open: out_2
  nor nor_2 (nor_2_out, Latch8_out, Latch9_out);
  nor nor_3 (nor_3_out, IRQP_Latch_out_2, not_26_out);
  not not_28 (not_28_out, nor_6_out);
  not not_29 (not_29_out, BLatch1_out);
  nor nor_4 (nor_4_out, Latch6_out, nor_5_out);
  nor nor_5 (nor_5_out, Latch11_out, Latch12_out);
  nor nor_6 (nor_6_out, LastLatch_out, nor_2_out);
  nor nor_7 (nor_7_out, Latch4_out, Latch5_out);
  or or_1 (or_1_out, nor_3_out, not_28_out);
  D_LATCH BLatch2 (.EN(PHI0), .in(and_11_out), .out(BLatch2_out));  // open: out_2
  and and_11 (and_11_out, or_2_out, not_29_out);
  nor nor_8 (nor_8_out, Latch7_out_2, not_15_out, nor_4_out);
  not not_30 (DORES, nor_7_out);
  nor nor_9 (nor_9_out, nor_7_out, BRK6E);
  nor nor_10 (nor_10_out, BR2, T0);
  not not_31 (not_31_out, or_1_out);
  not not_32 (not_32_out, PHI0);
  or or_2 (or_2_out, nor_10_out, not_31_out);
  nor nor_11 (nor_11_out, BLatch2_out, BRK6E);
  D_LATCH LastLatch (.EN(not_32_out), .in(nor_8_out), .out(LastLatch_out));  // open: out_2
  nor nor_12 (B_OUT, DORES, nor_11_out);
  not not_33 (not_33_out, BRK5);
  or or_3 (or_3_out, nor_1_out, not_34_out);
  not not_34 (not_34_out, DORES);
  nor nor_13 (nor_13_out, nor_1_out, nor_6_out, DORES);
  D_LATCH ADL0_Latch (.EN(PHI0), .in(not_33_out), .out_2(_0_ADL0));  // open: out
  D_LATCH ADL1_Latch (.EN(PHI0), .in(or_3_out), .out_2(_0_ADL1));  // open: out
  D_LATCH ADL2_Latch (.EN(PHI0), .in(nor_13_out), .out_2(ADL2_Latch_out_2));  // open: out
  not not_35 (_0_ADL2, ADL2_Latch_out_2);

  // Notes on the sheet:
  //   6502 INTERRUPT HANDLING
  //   INPUT TRIGGERS
  //   INTERRUPT CYCLE 6-7
  //   /NMIP
  //   /IRQP
  //   RESP
  //   /ready
  //   BRK6E
  //   BRK7
  //   BRK6E
  //   BRK7
  //   /I_OUT
  //   BRK6E
  //   NMI EDGE DETECT
  //   /IRQP
  //   /DONMI
  //   B FLAG
  //   RESET FLIP/FLOP
  //   BRK6E
  //   BR2
  //   T0
  //   INTERRUPT CHECK
  //   /DONMI
  //   DORES
  //   BRK5
  //   BRK7
  //   INTERRUPT ADDRESS
endmodule
module DECODER_TRANS (
  input  nT5,
  input  nT4,
  input  nT3,
  input  nT2,
  input  IR0,
  input  IR1,
  input  IR7,
  input  IR4,
  input  IR3,
  input  IR2,
  input  IR6,
  input  IR5,
  input  nT0X,
  input  nT1X,
  output _0,
  output _1,
  output _2,
  output _3,
  output _4,
  output _5,
  output _6,
  output _7,
  output _8,
  output _9,
  output _10,
  output _11,
  output _12,
  output _13,
  output _14,
  output _15,
  output _16,
  output _17,
  output _18,
  output _19,
  output _20,
  output _21,
  output _22,
  output _23,
  output _24,
  output _25,
  output _26,
  output _27,
  output _28,
  output _29,
  output _30,
  output _31,
  output _32,
  output _33,
  output _34,
  output _35,
  output _36,
  output _37,
  output _38,
  output _39,
  output _40,
  output _41,
  output _42,
  output _43,
  output _44,
  output _45,
  output _46,
  output _47,
  output _48,
  output _49,
  output _50,
  output _51,
  output _52,
  output _53,
  output _54,
  output _55,
  output _56,
  output _57,
  output _58,
  output _59,
  output _60,
  output _61,
  output _62,
  output _63,
  output _64,
  output _65,
  output _66,
  output _67,
  output _68,
  output _69,
  output _70,
  output _71,
  output _72,
  output _73,
  output _74,
  output _75,
  output _76,
  output _77,
  output _78,
  output _79,
  output _80,
  output _81,
  output _82,
  output _83,
  output _84,
  output _85,
  output _86,
  output _87,
  output _88,
  output _89,
  output _90,
  output _91,
  output _92,
  output _93,
  output _94,
  output _95,
  output _96,
  output _97,
  output _98,
  output _99,
  output _100,
  output _101,
  output _102,
  output _103,
  output _104,
  output _105,
  output _106,
  output _107,
  output _108,
  output _109,
  output _110,
  output _111,
  output _112,
  output _113,
  output _114,
  output _115,
  output _116,
  output _117,
  output _118,
  output _119,
  output _120,
  output _121,
  output _122,
  output _123,
  output _124,
  output _125,
  output _126,
  output _127,
  output _128,
  output _129
);

  wire not_1_out, not_2_out, not_3_out, not_4_out, not_5_out, not_6_out, not_7_out, not_8_out, or_1_out;

  not not_1 (not_1_out, IR1);
  or or_1 (or_1_out, IR0, IR1);
  not not_2 (not_2_out, IR0);
  not not_3 (not_3_out, IR7);
  not not_4 (not_4_out, IR4);
  not not_5 (not_5_out, IR3);
  not not_6 (not_6_out, IR2);
  not not_7 (not_7_out, IR6);
  not not_8 (not_8_out, IR5);
  Pull_Resistor #(.pull(1)) pull_resistor_1 (.node(_0));
  Pull_Resistor #(.pull(1)) pull_resistor_2 (.node(_1));
  Transistor #(.\type ("n")) transistor_1 (.in(1'b0), .out(_1), .gate(nT3));
  Transistor #(.\type ("n")) transistor_2 (.in(1'b0), .out(_0), .gate(or_1_out));
  Transistor #(.\type ("n")) transistor_3 (.in(1'b0), .out(_1), .gate(not_2_out));
  Transistor #(.\type ("n")) transistor_4 (.in(1'b0), .out(_0), .gate(not_3_out));
  Transistor #(.\type ("n")) transistor_5 (.in(1'b0), .out(_1), .gate(not_4_out));
  Transistor #(.\type ("n")) transistor_6 (.in(1'b0), .out(_1), .gate(IR3));
  Transistor #(.\type ("n")) transistor_7 (.in(1'b0), .out(_1), .gate(IR2));
  Transistor #(.\type ("n")) transistor_8 (.in(1'b0), .out(_0), .gate(not_6_out));
  Transistor #(.\type ("n")) transistor_9 (.in(1'b0), .out(_0), .gate(IR6));
  Transistor #(.\type ("n")) transistor_10 (.in(1'b0), .out(_0), .gate(IR5));
  Pull_Resistor #(.pull(1)) pull_resistor_3 (.node(_2));
  Transistor #(.\type ("n")) transistor_11 (.in(1'b0), .out(_2), .gate(nT2));
  Transistor #(.\type ("n")) transistor_12 (.in(1'b0), .out(_2), .gate(not_2_out));
  Transistor #(.\type ("n")) transistor_13 (.in(1'b0), .out(_2), .gate(not_4_out));
  Transistor #(.\type ("n")) transistor_14 (.in(1'b0), .out(_2), .gate(not_5_out));
  Transistor #(.\type ("n")) transistor_15 (.in(1'b0), .out(_2), .gate(IR2));
  Pull_Resistor #(.pull(1)) pull_resistor_4 (.node(_3));
  Transistor #(.\type ("n")) transistor_16 (.in(1'b0), .out(_3), .gate(or_1_out));
  Transistor #(.\type ("n")) transistor_17 (.in(1'b0), .out(_3), .gate(not_3_out));
  Transistor #(.\type ("n")) transistor_18 (.in(1'b0), .out(_3), .gate(IR4));
  Transistor #(.\type ("n")) transistor_19 (.in(1'b0), .out(_3), .gate(not_5_out));
  Transistor #(.\type ("n")) transistor_20 (.in(1'b0), .out(_3), .gate(IR2));
  Transistor #(.\type ("n")) transistor_21 (.in(1'b0), .out(_3), .gate(IR5));
  Transistor #(.\type ("n")) transistor_22 (.in(1'b0), .out(_3), .gate(nT0X));
  Pull_Resistor #(.pull(1)) pull_resistor_5 (.node(_4));
  Pull_Resistor #(.pull(1)) pull_resistor_6 (.node(_5));
  Transistor #(.\type ("n")) transistor_23 (.in(1'b0), .out(_5), .gate(or_1_out));
  Transistor #(.\type ("n")) transistor_24 (.in(1'b0), .out(_4), .gate(or_1_out));
  Transistor #(.\type ("n")) transistor_25 (.in(1'b0), .out(_5), .gate(not_3_out));
  Transistor #(.\type ("n")) transistor_26 (.in(1'b0), .out(_4), .gate(not_3_out));
  Transistor #(.\type ("n")) transistor_27 (.in(1'b0), .out(_5), .gate(IR4));
  Transistor #(.\type ("n")) transistor_28 (.in(1'b0), .out(_4), .gate(not_4_out));
  Transistor #(.\type ("n")) transistor_29 (.in(1'b0), .out(_4), .gate(not_5_out));
  Transistor #(.\type ("n")) transistor_30 (.in(1'b0), .out(_4), .gate(IR2));
  Transistor #(.\type ("n")) transistor_31 (.in(1'b0), .out(_4), .gate(IR6));
  Transistor #(.\type ("n")) transistor_32 (.in(1'b0), .out(_5), .gate(not_7_out));
  Transistor #(.\type ("n")) transistor_33 (.in(1'b0), .out(_4), .gate(IR5));
  Transistor #(.\type ("n")) transistor_34 (.in(1'b0), .out(_5), .gate(IR5));
  Transistor #(.\type ("n")) transistor_35 (.in(1'b0), .out(_5), .gate(nT0X));
  Transistor #(.\type ("n")) transistor_36 (.in(1'b0), .out(_4), .gate(nT0X));
  Pull_Resistor #(.pull(1)) pull_resistor_7 (.node(_6));
  Transistor #(.\type ("n")) transistor_37 (.in(1'b0), .out(_6), .gate(nT2));
  Transistor #(.\type ("n")) transistor_38 (.in(1'b0), .out(_6), .gate(not_4_out));
  Transistor #(.\type ("n")) transistor_39 (.in(1'b0), .out(_6), .gate(not_6_out));
  Pull_Resistor #(.pull(1)) pull_resistor_8 (.node(_7));
  Transistor #(.\type ("n")) transistor_40 (.in(1'b0), .out(_7), .gate(not_1_out));
  Transistor #(.\type ("n")) transistor_41 (.in(1'b0), .out(_7), .gate(not_3_out));
  Transistor #(.\type ("n")) transistor_42 (.in(1'b0), .out(_7), .gate(IR6));
  Pull_Resistor #(.pull(1)) pull_resistor_9 (.node(_9));
  Pull_Resistor #(.pull(1)) pull_resistor_10 (.node(_8));
  Transistor #(.\type ("n")) transistor_43 (.in(1'b0), .out(_8), .gate(nT2));
  Transistor #(.\type ("n")) transistor_44 (.in(1'b0), .out(_9), .gate(not_1_out));
  Transistor #(.\type ("n")) transistor_45 (.in(1'b0), .out(_8), .gate(not_2_out));
  Transistor #(.\type ("n")) transistor_46 (.in(1'b0), .out(_9), .gate(not_3_out));
  Transistor #(.\type ("n")) transistor_47 (.in(1'b0), .out(_9), .gate(IR4));
  Transistor #(.\type ("n")) transistor_48 (.in(1'b0), .out(_8), .gate(IR4));
  Transistor #(.\type ("n")) transistor_49 (.in(1'b0), .out(_8), .gate(IR3));
  Transistor #(.\type ("n")) transistor_50 (.in(1'b0), .out(_9), .gate(not_5_out));
  Transistor #(.\type ("n")) transistor_51 (.in(1'b0), .out(_9), .gate(IR2));
  Transistor #(.\type ("n")) transistor_52 (.in(1'b0), .out(_8), .gate(IR2));
  Transistor #(.\type ("n")) transistor_53 (.in(1'b0), .out(_9), .gate(IR6));
  Transistor #(.\type ("n")) transistor_54 (.in(1'b0), .out(_9), .gate(IR5));
  Transistor #(.\type ("n")) transistor_55 (.in(1'b0), .out(_9), .gate(nT0X));
  Pull_Resistor #(.pull(1)) pull_resistor_11 (.node(_10));
  Transistor #(.\type ("n")) transistor_56 (.in(1'b0), .out(_10), .gate(not_1_out));
  Transistor #(.\type ("n")) transistor_57 (.in(1'b0), .out(_10), .gate(not_3_out));
  Transistor #(.\type ("n")) transistor_58 (.in(1'b0), .out(_10), .gate(IR4));
  Transistor #(.\type ("n")) transistor_59 (.in(1'b0), .out(_10), .gate(not_5_out));
  Transistor #(.\type ("n")) transistor_60 (.in(1'b0), .out(_10), .gate(IR2));
  Transistor #(.\type ("n")) transistor_61 (.in(1'b0), .out(_10), .gate(not_7_out));
  Transistor #(.\type ("n")) transistor_62 (.in(1'b0), .out(_10), .gate(IR5));
  Transistor #(.\type ("n")) transistor_63 (.in(1'b0), .out(_10), .gate(nT0X));
  Pull_Resistor #(.pull(1)) pull_resistor_12 (.node(_11));
  Transistor #(.\type ("n")) transistor_64 (.in(1'b0), .out(_11), .gate(or_1_out));
  Transistor #(.\type ("n")) transistor_65 (.in(1'b0), .out(_11), .gate(not_3_out));
  Transistor #(.\type ("n")) transistor_66 (.in(1'b0), .out(_11), .gate(IR4));
  Transistor #(.\type ("n")) transistor_67 (.in(1'b0), .out(_11), .gate(not_7_out));
  Transistor #(.\type ("n")) transistor_68 (.in(1'b0), .out(_11), .gate(not_8_out));
  Transistor #(.\type ("n")) transistor_69 (.in(1'b0), .out(_11), .gate(nT0X));
  Pull_Resistor #(.pull(1)) pull_resistor_13 (.node(_13));
  Pull_Resistor #(.pull(1)) pull_resistor_14 (.node(_12));
  Transistor #(.\type ("n")) transistor_70 (.in(1'b0), .out(_12), .gate(not_1_out));
  Transistor #(.\type ("n")) transistor_71 (.in(1'b0), .out(_13), .gate(not_1_out));
  Transistor #(.\type ("n")) transistor_72 (.in(1'b0), .out(_12), .gate(not_3_out));
  Transistor #(.\type ("n")) transistor_73 (.in(1'b0), .out(_13), .gate(not_3_out));
  Transistor #(.\type ("n")) transistor_74 (.in(1'b0), .out(_13), .gate(not_4_out));
  Transistor #(.\type ("n")) transistor_75 (.in(1'b0), .out(_13), .gate(not_5_out));
  Transistor #(.\type ("n")) transistor_76 (.in(1'b0), .out(_13), .gate(IR2));
  Transistor #(.\type ("n")) transistor_77 (.in(1'b0), .out(_13), .gate(IR6));
  Transistor #(.\type ("n")) transistor_78 (.in(1'b0), .out(_12), .gate(IR6));
  Transistor #(.\type ("n")) transistor_79 (.in(1'b0), .out(_13), .gate(IR5));
  Transistor #(.\type ("n")) transistor_80 (.in(1'b0), .out(_12), .gate(IR5));
  Transistor #(.\type ("n")) transistor_81 (.in(1'b0), .out(_13), .gate(nT0X));
  Pull_Resistor #(.pull(1)) pull_resistor_15 (.node(_14));
  Transistor #(.\type ("n")) transistor_82 (.in(1'b0), .out(_14), .gate(not_1_out));
  Transistor #(.\type ("n")) transistor_83 (.in(1'b0), .out(_14), .gate(not_3_out));
  Transistor #(.\type ("n")) transistor_84 (.in(1'b0), .out(_14), .gate(IR6));
  Transistor #(.\type ("n")) transistor_85 (.in(1'b0), .out(_14), .gate(not_8_out));
  Transistor #(.\type ("n")) transistor_86 (.in(1'b0), .out(_14), .gate(nT0X));
  Pull_Resistor #(.pull(1)) pull_resistor_16 (.node(_15));
  Transistor #(.\type ("n")) transistor_87 (.in(1'b0), .out(_15), .gate(not_1_out));
  Transistor #(.\type ("n")) transistor_88 (.in(1'b0), .out(_15), .gate(not_3_out));
  Transistor #(.\type ("n")) transistor_89 (.in(1'b0), .out(_15), .gate(IR4));
  Transistor #(.\type ("n")) transistor_90 (.in(1'b0), .out(_15), .gate(not_5_out));
  Transistor #(.\type ("n")) transistor_91 (.in(1'b0), .out(_15), .gate(IR2));
  Transistor #(.\type ("n")) transistor_92 (.in(1'b0), .out(_15), .gate(not_7_out));
  Transistor #(.\type ("n")) transistor_93 (.in(1'b0), .out(_15), .gate(IR5));
  Transistor #(.\type ("n")) transistor_94 (.in(1'b0), .out(_15), .gate(nT1X));
  Pull_Resistor #(.pull(1)) pull_resistor_17 (.node(_16));
  Pull_Resistor #(.pull(1)) pull_resistor_18 (.node(_17));
  Transistor #(.\type ("n")) transistor_95 (.in(1'b0), .out(_17), .gate(not_1_out));
  Transistor #(.\type ("n")) transistor_96 (.in(1'b0), .out(_16), .gate(or_1_out));
  Transistor #(.\type ("n")) transistor_97 (.in(1'b0), .out(_17), .gate(not_3_out));
  Transistor #(.\type ("n")) transistor_98 (.in(1'b0), .out(_16), .gate(not_3_out));
  Transistor #(.\type ("n")) transistor_99 (.in(1'b0), .out(_16), .gate(IR4));
  Transistor #(.\type ("n")) transistor_100 (.in(1'b0), .out(_17), .gate(not_4_out));
  Transistor #(.\type ("n")) transistor_101 (.in(1'b0), .out(_16), .gate(not_5_out));
  Transistor #(.\type ("n")) transistor_102 (.in(1'b0), .out(_17), .gate(not_5_out));
  Transistor #(.\type ("n")) transistor_103 (.in(1'b0), .out(_17), .gate(IR2));
  Transistor #(.\type ("n")) transistor_104 (.in(1'b0), .out(_16), .gate(IR2));
  Transistor #(.\type ("n")) transistor_105 (.in(1'b0), .out(_17), .gate(IR6));
  Transistor #(.\type ("n")) transistor_106 (.in(1'b0), .out(_16), .gate(not_7_out));
  Transistor #(.\type ("n")) transistor_107 (.in(1'b0), .out(_16), .gate(not_8_out));
  Transistor #(.\type ("n")) transistor_108 (.in(1'b0), .out(_17), .gate(not_8_out));
  Transistor #(.\type ("n")) transistor_109 (.in(1'b0), .out(_17), .gate(nT0X));
  Transistor #(.\type ("n")) transistor_110 (.in(1'b0), .out(_16), .gate(nT1X));
  Pull_Resistor #(.pull(1)) pull_resistor_19 (.node(_18));
  Transistor #(.\type ("n")) transistor_111 (.in(1'b0), .out(_18), .gate(or_1_out));
  Transistor #(.\type ("n")) transistor_112 (.in(1'b0), .out(_18), .gate(not_3_out));
  Transistor #(.\type ("n")) transistor_113 (.in(1'b0), .out(_18), .gate(IR4));
  Transistor #(.\type ("n")) transistor_114 (.in(1'b0), .out(_18), .gate(not_5_out));
  Transistor #(.\type ("n")) transistor_115 (.in(1'b0), .out(_18), .gate(IR2));
  Transistor #(.\type ("n")) transistor_116 (.in(1'b0), .out(_18), .gate(IR5));
  Transistor #(.\type ("n")) transistor_117 (.in(1'b0), .out(_18), .gate(nT1X));
  Pull_Resistor #(.pull(1)) pull_resistor_20 (.node(_19));
  Transistor #(.\type ("n")) transistor_118 (.in(1'b0), .out(_19), .gate(or_1_out));
  Transistor #(.\type ("n")) transistor_119 (.in(1'b0), .out(_19), .gate(not_3_out));
  Transistor #(.\type ("n")) transistor_120 (.in(1'b0), .out(_19), .gate(not_6_out));
  Transistor #(.\type ("n")) transistor_121 (.in(1'b0), .out(_19), .gate(IR6));
  Transistor #(.\type ("n")) transistor_122 (.in(1'b0), .out(_19), .gate(not_8_out));
  Transistor #(.\type ("n")) transistor_123 (.in(1'b0), .out(_19), .gate(nT0X));
  Pull_Resistor #(.pull(1)) pull_resistor_21 (.node(_20));
  Transistor #(.\type ("n")) transistor_124 (.in(1'b0), .out(_20), .gate(or_1_out));
  Transistor #(.\type ("n")) transistor_125 (.in(1'b0), .out(_20), .gate(not_3_out));
  Transistor #(.\type ("n")) transistor_126 (.in(1'b0), .out(_20), .gate(IR4));
  Transistor #(.\type ("n")) transistor_127 (.in(1'b0), .out(_20), .gate(IR6));
  Transistor #(.\type ("n")) transistor_128 (.in(1'b0), .out(_20), .gate(not_8_out));
  Transistor #(.\type ("n")) transistor_129 (.in(1'b0), .out(_20), .gate(nT0X));
  Pull_Resistor #(.pull(1)) pull_resistor_22 (.node(_21));
  Transistor #(.\type ("n")) transistor_130 (.in(1'b0), .out(_21), .gate(or_1_out));
  Transistor #(.\type ("n")) transistor_131 (.in(1'b0), .out(_21), .gate(IR7));
  Transistor #(.\type ("n")) transistor_132 (.in(1'b0), .out(_21), .gate(IR4));
  Transistor #(.\type ("n")) transistor_133 (.in(1'b0), .out(_21), .gate(IR3));
  Transistor #(.\type ("n")) transistor_134 (.in(1'b0), .out(_21), .gate(IR2));
  Transistor #(.\type ("n")) transistor_135 (.in(1'b0), .out(_21), .gate(IR6));
  Transistor #(.\type ("n")) transistor_136 (.in(1'b0), .out(_21), .gate(not_8_out));
  Transistor #(.\type ("n")) transistor_137 (.in(1'b0), .out(_21), .gate(nT0X));
  Pull_Resistor #(.pull(1)) pull_resistor_23 (.node(_22));
  Transistor #(.\type ("n")) transistor_138 (.in(1'b0), .out(_22), .gate(nT5));
  Transistor #(.\type ("n")) transistor_139 (.in(1'b0), .out(_22), .gate(or_1_out));
  Transistor #(.\type ("n")) transistor_140 (.in(1'b0), .out(_22), .gate(IR7));
  Transistor #(.\type ("n")) transistor_141 (.in(1'b0), .out(_22), .gate(IR4));
  Transistor #(.\type ("n")) transistor_142 (.in(1'b0), .out(_22), .gate(IR3));
  Transistor #(.\type ("n")) transistor_143 (.in(1'b0), .out(_22), .gate(IR2));
  Transistor #(.\type ("n")) transistor_144 (.in(1'b0), .out(_22), .gate(IR6));
  Transistor #(.\type ("n")) transistor_145 (.in(1'b0), .out(_22), .gate(IR5));
  Pull_Resistor #(.pull(1)) pull_resistor_24 (.node(_23));
  Transistor #(.\type ("n")) transistor_146 (.in(1'b0), .out(_23), .gate(or_1_out));
  Transistor #(.\type ("n")) transistor_147 (.in(1'b0), .out(_23), .gate(IR7));
  Transistor #(.\type ("n")) transistor_148 (.in(1'b0), .out(_23), .gate(IR4));
  Transistor #(.\type ("n")) transistor_149 (.in(1'b0), .out(_23), .gate(not_5_out));
  Transistor #(.\type ("n")) transistor_150 (.in(1'b0), .out(_23), .gate(IR2));
  Transistor #(.\type ("n")) transistor_151 (.in(1'b0), .out(_23), .gate(IR5));
  Transistor #(.\type ("n")) transistor_152 (.in(1'b0), .out(_23), .gate(nT0X));
  Pull_Resistor #(.pull(1)) pull_resistor_25 (.node(_24));
  Pull_Resistor #(.pull(1)) pull_resistor_26 (.node(_25));
  Transistor #(.\type ("n")) transistor_153 (.in(1'b0), .out(_24), .gate(nT4));
  Transistor #(.\type ("n")) transistor_154 (.in(1'b0), .out(_25), .gate(nT3));
  Transistor #(.\type ("n")) transistor_155 (.in(1'b0), .out(_24), .gate(or_1_out));
  Transistor #(.\type ("n")) transistor_156 (.in(1'b0), .out(_25), .gate(or_1_out));
  Transistor #(.\type ("n")) transistor_157 (.in(1'b0), .out(_24), .gate(IR7));
  Transistor #(.\type ("n")) transistor_158 (.in(1'b0), .out(_25), .gate(IR7));
  Transistor #(.\type ("n")) transistor_159 (.in(1'b0), .out(_24), .gate(IR4));
  Transistor #(.\type ("n")) transistor_160 (.in(1'b0), .out(_25), .gate(IR4));
  Transistor #(.\type ("n")) transistor_161 (.in(1'b0), .out(_24), .gate(IR3));
  Transistor #(.\type ("n")) transistor_162 (.in(1'b0), .out(_25), .gate(not_5_out));
  Transistor #(.\type ("n")) transistor_163 (.in(1'b0), .out(_24), .gate(IR2));
  Transistor #(.\type ("n")) transistor_164 (.in(1'b0), .out(_25), .gate(IR2));
  Transistor #(.\type ("n")) transistor_165 (.in(1'b0), .out(_24), .gate(not_7_out));
  Transistor #(.\type ("n")) transistor_166 (.in(1'b0), .out(_25), .gate(not_8_out));
  Transistor #(.\type ("n")) transistor_167 (.in(1'b0), .out(_24), .gate(not_8_out));
  Pull_Resistor #(.pull(1)) pull_resistor_27 (.node(_26));
  Transistor #(.\type ("n")) transistor_168 (.in(1'b0), .out(_26), .gate(nT5));
  Transistor #(.\type ("n")) transistor_169 (.in(1'b0), .out(_26), .gate(or_1_out));
  Transistor #(.\type ("n")) transistor_170 (.in(1'b0), .out(_26), .gate(IR7));
  Transistor #(.\type ("n")) transistor_171 (.in(1'b0), .out(_26), .gate(IR4));
  Transistor #(.\type ("n")) transistor_172 (.in(1'b0), .out(_26), .gate(IR3));
  Transistor #(.\type ("n")) transistor_173 (.in(1'b0), .out(_26), .gate(IR2));
  Transistor #(.\type ("n")) transistor_174 (.in(1'b0), .out(_26), .gate(not_7_out));
  Transistor #(.\type ("n")) transistor_175 (.in(1'b0), .out(_26), .gate(IR5));
  Pull_Resistor #(.pull(1)) pull_resistor_28 (.node(_27));
  Transistor #(.\type ("n")) transistor_176 (.in(1'b0), .out(_27), .gate(not_1_out));
  Transistor #(.\type ("n")) transistor_177 (.in(1'b0), .out(_27), .gate(IR7));
  Transistor #(.\type ("n")) transistor_178 (.in(1'b0), .out(_27), .gate(not_7_out));
  Transistor #(.\type ("n")) transistor_179 (.in(1'b0), .out(_27), .gate(not_8_out));
  Pull_Resistor #(.pull(1)) pull_resistor_29 (.node(_28));
  Pull_Resistor #(.pull(1)) pull_resistor_30 (.node(_29));
  Transistor #(.\type ("n")) transistor_180 (.in(1'b0), .out(_28), .gate(nT2));
  Transistor #(.\type ("n")) transistor_181 (.in(1'b0), .out(_29), .gate(not_2_out));
  Transistor #(.\type ("n")) transistor_182 (.in(1'b0), .out(_29), .gate(IR7));
  Transistor #(.\type ("n")) transistor_183 (.in(1'b0), .out(_29), .gate(not_7_out));
  Transistor #(.\type ("n")) transistor_184 (.in(1'b0), .out(_29), .gate(IR5));
  Transistor #(.\type ("n")) transistor_185 (.in(1'b0), .out(_29), .gate(nT0X));
  Pull_Resistor #(.pull(1)) pull_resistor_31 (.node(_30));
  Transistor #(.\type ("n")) transistor_186 (.in(1'b0), .out(_30), .gate(or_1_out));
  Transistor #(.\type ("n")) transistor_187 (.in(1'b0), .out(_30), .gate(IR7));
  Transistor #(.\type ("n")) transistor_188 (.in(1'b0), .out(_30), .gate(IR4));
  Transistor #(.\type ("n")) transistor_189 (.in(1'b0), .out(_30), .gate(not_5_out));
  Transistor #(.\type ("n")) transistor_190 (.in(1'b0), .out(_30), .gate(not_6_out));
  Transistor #(.\type ("n")) transistor_191 (.in(1'b0), .out(_30), .gate(not_7_out));
  Pull_Resistor #(.pull(1)) pull_resistor_32 (.node(_31));
  Transistor #(.\type ("n")) transistor_192 (.in(1'b0), .out(_31), .gate(nT2));
  Transistor #(.\type ("n")) transistor_193 (.in(1'b0), .out(_31), .gate(IR4));
  Transistor #(.\type ("n")) transistor_194 (.in(1'b0), .out(_31), .gate(not_5_out));
  Transistor #(.\type ("n")) transistor_195 (.in(1'b0), .out(_31), .gate(not_6_out));
  Pull_Resistor #(.pull(1)) pull_resistor_33 (.node(_32));
  Pull_Resistor #(.pull(1)) pull_resistor_34 (.node(_33));
  Transistor #(.\type ("n")) transistor_196 (.in(1'b0), .out(_33), .gate(nT2));
  Transistor #(.\type ("n")) transistor_197 (.in(1'b0), .out(_32), .gate(not_2_out));
  Transistor #(.\type ("n")) transistor_198 (.in(1'b0), .out(_32), .gate(IR7));
  Transistor #(.\type ("n")) transistor_199 (.in(1'b0), .out(_33), .gate(IR3));
  Transistor #(.\type ("n")) transistor_200 (.in(1'b0), .out(_32), .gate(IR6));
  Transistor #(.\type ("n")) transistor_201 (.in(1'b0), .out(_32), .gate(IR5));
  Transistor #(.\type ("n")) transistor_202 (.in(1'b0), .out(_32), .gate(nT0X));
  Pull_Resistor #(.pull(1)) pull_resistor_35 (.node(_34));
  Transistor #(.\type ("n")) transistor_203 (.in(1'b0), .out(_34), .gate(nT0X));
  Pull_Resistor #(.pull(1)) pull_resistor_36 (.node(_35));
  Transistor #(.\type ("n")) transistor_204 (.in(1'b0), .out(_35), .gate(nT2));
  Transistor #(.\type ("n")) transistor_205 (.in(1'b0), .out(_35), .gate(or_1_out));
  Transistor #(.\type ("n")) transistor_206 (.in(1'b0), .out(_35), .gate(IR7));
  Transistor #(.\type ("n")) transistor_207 (.in(1'b0), .out(_35), .gate(IR4));
  Transistor #(.\type ("n")) transistor_208 (.in(1'b0), .out(_35), .gate(IR2));
  Pull_Resistor #(.pull(1)) pull_resistor_37 (.node(_36));
  Transistor #(.\type ("n")) transistor_209 (.in(1'b0), .out(_36), .gate(nT3));
  Transistor #(.\type ("n")) transistor_210 (.in(1'b0), .out(_36), .gate(or_1_out));
  Transistor #(.\type ("n")) transistor_211 (.in(1'b0), .out(_36), .gate(IR7));
  Transistor #(.\type ("n")) transistor_212 (.in(1'b0), .out(_36), .gate(IR4));
  Pull_Resistor #(.pull(1)) pull_resistor_38 (.node(_37));
  Transistor #(.\type ("n")) transistor_213 (.in(1'b0), .out(_37), .gate(nT4));
  Transistor #(.\type ("n")) transistor_214 (.in(1'b0), .out(_37), .gate(or_1_out));
  Transistor #(.\type ("n")) transistor_215 (.in(1'b0), .out(_37), .gate(IR7));
  Transistor #(.\type ("n")) transistor_216 (.in(1'b0), .out(_37), .gate(IR4));
  Transistor #(.\type ("n")) transistor_217 (.in(1'b0), .out(_37), .gate(IR3));
  Transistor #(.\type ("n")) transistor_218 (.in(1'b0), .out(_37), .gate(IR2));
  Transistor #(.\type ("n")) transistor_219 (.in(1'b0), .out(_37), .gate(IR6));
  Pull_Resistor #(.pull(1)) pull_resistor_39 (.node(_38));
  Transistor #(.\type ("n")) transistor_220 (.in(1'b0), .out(_38), .gate(nT4));
  Transistor #(.\type ("n")) transistor_221 (.in(1'b0), .out(_38), .gate(or_1_out));
  Transistor #(.\type ("n")) transistor_222 (.in(1'b0), .out(_38), .gate(IR7));
  Transistor #(.\type ("n")) transistor_223 (.in(1'b0), .out(_38), .gate(IR4));
  Transistor #(.\type ("n")) transistor_224 (.in(1'b0), .out(_38), .gate(IR3));
  Transistor #(.\type ("n")) transistor_225 (.in(1'b0), .out(_38), .gate(IR2));
  Transistor #(.\type ("n")) transistor_226 (.in(1'b0), .out(_38), .gate(not_7_out));
  Transistor #(.\type ("n")) transistor_227 (.in(1'b0), .out(_38), .gate(IR5));
  Pull_Resistor #(.pull(1)) pull_resistor_40 (.node(_40));
  Pull_Resistor #(.pull(1)) pull_resistor_41 (.node(_39));
  Transistor #(.\type ("n")) transistor_228 (.in(1'b0), .out(_40), .gate(nT4));
  Transistor #(.\type ("n")) transistor_229 (.in(1'b0), .out(_39), .gate(nT3));
  Transistor #(.\type ("n")) transistor_230 (.in(1'b0), .out(_40), .gate(not_2_out));
  Transistor #(.\type ("n")) transistor_231 (.in(1'b0), .out(_39), .gate(not_2_out));
  Transistor #(.\type ("n")) transistor_232 (.in(1'b0), .out(_39), .gate(IR4));
  Transistor #(.\type ("n")) transistor_233 (.in(1'b0), .out(_40), .gate(not_4_out));
  Transistor #(.\type ("n")) transistor_234 (.in(1'b0), .out(_40), .gate(IR3));
  Transistor #(.\type ("n")) transistor_235 (.in(1'b0), .out(_39), .gate(IR3));
  Transistor #(.\type ("n")) transistor_236 (.in(1'b0), .out(_39), .gate(IR2));
  Transistor #(.\type ("n")) transistor_237 (.in(1'b0), .out(_40), .gate(IR2));
  Pull_Resistor #(.pull(1)) pull_resistor_42 (.node(_41));
  Transistor #(.\type ("n")) transistor_238 (.in(1'b0), .out(_41), .gate(nT2));
  Transistor #(.\type ("n")) transistor_239 (.in(1'b0), .out(_41), .gate(not_2_out));
  Transistor #(.\type ("n")) transistor_240 (.in(1'b0), .out(_41), .gate(not_4_out));
  Transistor #(.\type ("n")) transistor_241 (.in(1'b0), .out(_41), .gate(IR3));
  Transistor #(.\type ("n")) transistor_242 (.in(1'b0), .out(_41), .gate(IR2));
  Pull_Resistor #(.pull(1)) pull_resistor_43 (.node(_42));
  Transistor #(.\type ("n")) transistor_243 (.in(1'b0), .out(_42), .gate(nT3));
  Transistor #(.\type ("n")) transistor_244 (.in(1'b0), .out(_42), .gate(not_4_out));
  Transistor #(.\type ("n")) transistor_245 (.in(1'b0), .out(_42), .gate(not_5_out));
  Pull_Resistor #(.pull(1)) pull_resistor_44 (.node(_44));
  Pull_Resistor #(.pull(1)) pull_resistor_45 (.node(_43));
  Transistor #(.\type ("n")) transistor_246 (.in(1'b0), .out(_44), .gate(not_1_out));
  Transistor #(.\type ("n")) transistor_247 (.in(1'b0), .out(_43), .gate(or_1_out));
  Transistor #(.\type ("n")) transistor_248 (.in(1'b0), .out(_43), .gate(IR7));
  Transistor #(.\type ("n")) transistor_249 (.in(1'b0), .out(_44), .gate(not_3_out));
  Transistor #(.\type ("n")) transistor_250 (.in(1'b0), .out(_43), .gate(IR4));
  Transistor #(.\type ("n")) transistor_251 (.in(1'b0), .out(_43), .gate(not_5_out));
  Transistor #(.\type ("n")) transistor_252 (.in(1'b0), .out(_43), .gate(IR2));
  Transistor #(.\type ("n")) transistor_253 (.in(1'b0), .out(_44), .gate(not_7_out));
  Transistor #(.\type ("n")) transistor_254 (.in(1'b0), .out(_43), .gate(not_8_out));
  Transistor #(.\type ("n")) transistor_255 (.in(1'b0), .out(_44), .gate(not_8_out));
  Pull_Resistor #(.pull(1)) pull_resistor_46 (.node(_45));
  Transistor #(.\type ("n")) transistor_256 (.in(1'b0), .out(_45), .gate(nT4));
  Transistor #(.\type ("n")) transistor_257 (.in(1'b0), .out(_45), .gate(not_2_out));
  Transistor #(.\type ("n")) transistor_258 (.in(1'b0), .out(_45), .gate(IR4));
  Transistor #(.\type ("n")) transistor_259 (.in(1'b0), .out(_45), .gate(IR3));
  Transistor #(.\type ("n")) transistor_260 (.in(1'b0), .out(_45), .gate(IR2));
  Pull_Resistor #(.pull(1)) pull_resistor_47 (.node(_46));
  Transistor #(.\type ("n")) transistor_261 (.in(1'b0), .out(_46), .gate(nT3));
  Transistor #(.\type ("n")) transistor_262 (.in(1'b0), .out(_46), .gate(not_2_out));
  Transistor #(.\type ("n")) transistor_263 (.in(1'b0), .out(_46), .gate(not_4_out));
  Transistor #(.\type ("n")) transistor_264 (.in(1'b0), .out(_46), .gate(IR3));
  Transistor #(.\type ("n")) transistor_265 (.in(1'b0), .out(_46), .gate(IR2));
  Pull_Resistor #(.pull(1)) pull_resistor_48 (.node(_47));
  Pull_Resistor #(.pull(1)) pull_resistor_49 (.node(_48));
  Transistor #(.\type ("n")) transistor_266 (.in(1'b0), .out(_48), .gate(nT2));
  Transistor #(.\type ("n")) transistor_267 (.in(1'b0), .out(_48), .gate(or_1_out));
  Transistor #(.\type ("n")) transistor_268 (.in(1'b0), .out(_47), .gate(or_1_out));
  Transistor #(.\type ("n")) transistor_269 (.in(1'b0), .out(_48), .gate(IR7));
  Transistor #(.\type ("n")) transistor_270 (.in(1'b0), .out(_47), .gate(IR7));
  Transistor #(.\type ("n")) transistor_271 (.in(1'b0), .out(_47), .gate(IR4));
  Transistor #(.\type ("n")) transistor_272 (.in(1'b0), .out(_48), .gate(IR4));
  Transistor #(.\type ("n")) transistor_273 (.in(1'b0), .out(_48), .gate(IR3));
  Transistor #(.\type ("n")) transistor_274 (.in(1'b0), .out(_47), .gate(IR3));
  Transistor #(.\type ("n")) transistor_275 (.in(1'b0), .out(_47), .gate(IR2));
  Transistor #(.\type ("n")) transistor_276 (.in(1'b0), .out(_48), .gate(IR2));
  Transistor #(.\type ("n")) transistor_277 (.in(1'b0), .out(_48), .gate(IR6));
  Transistor #(.\type ("n")) transistor_278 (.in(1'b0), .out(_47), .gate(not_7_out));
  Transistor #(.\type ("n")) transistor_279 (.in(1'b0), .out(_48), .gate(not_8_out));
  Pull_Resistor #(.pull(1)) pull_resistor_50 (.node(_49));
  Transistor #(.\type ("n")) transistor_280 (.in(1'b0), .out(_49), .gate(or_1_out));
  Transistor #(.\type ("n")) transistor_281 (.in(1'b0), .out(_49), .gate(not_3_out));
  Transistor #(.\type ("n")) transistor_282 (.in(1'b0), .out(_49), .gate(IR4));
  Transistor #(.\type ("n")) transistor_283 (.in(1'b0), .out(_49), .gate(not_7_out));
  Transistor #(.\type ("n")) transistor_284 (.in(1'b0), .out(_49), .gate(nT0X));
  Pull_Resistor #(.pull(1)) pull_resistor_51 (.node(_50));
  Transistor #(.\type ("n")) transistor_285 (.in(1'b0), .out(_50), .gate(not_2_out));
  Transistor #(.\type ("n")) transistor_286 (.in(1'b0), .out(_50), .gate(not_3_out));
  Transistor #(.\type ("n")) transistor_287 (.in(1'b0), .out(_50), .gate(not_7_out));
  Transistor #(.\type ("n")) transistor_288 (.in(1'b0), .out(_50), .gate(IR5));
  Transistor #(.\type ("n")) transistor_289 (.in(1'b0), .out(_50), .gate(nT0X));
  Pull_Resistor #(.pull(1)) pull_resistor_52 (.node(_52));
  Pull_Resistor #(.pull(1)) pull_resistor_53 (.node(_51));
  Transistor #(.\type ("n")) transistor_290 (.in(1'b0), .out(_52), .gate(not_2_out));
  Transistor #(.\type ("n")) transistor_291 (.in(1'b0), .out(_51), .gate(not_2_out));
  Transistor #(.\type ("n")) transistor_292 (.in(1'b0), .out(_51), .gate(not_3_out));
  Transistor #(.\type ("n")) transistor_293 (.in(1'b0), .out(_52), .gate(not_7_out));
  Transistor #(.\type ("n")) transistor_294 (.in(1'b0), .out(_51), .gate(not_7_out));
  Transistor #(.\type ("n")) transistor_295 (.in(1'b0), .out(_51), .gate(not_8_out));
  Transistor #(.\type ("n")) transistor_296 (.in(1'b0), .out(_52), .gate(not_8_out));
  Transistor #(.\type ("n")) transistor_297 (.in(1'b0), .out(_51), .gate(nT0X));
  Transistor #(.\type ("n")) transistor_298 (.in(1'b0), .out(_52), .gate(nT0X));
  Pull_Resistor #(.pull(1)) pull_resistor_54 (.node(_53));
  Transistor #(.\type ("n")) transistor_299 (.in(1'b0), .out(_53), .gate(not_1_out));
  Transistor #(.\type ("n")) transistor_300 (.in(1'b0), .out(_53), .gate(IR7));
  Transistor #(.\type ("n")) transistor_301 (.in(1'b0), .out(_53), .gate(IR6));
  Transistor #(.\type ("n")) transistor_302 (.in(1'b0), .out(_53), .gate(not_8_out));
  Pull_Resistor #(.pull(1)) pull_resistor_55 (.node(_54));
  Transistor #(.\type ("n")) transistor_303 (.in(1'b0), .out(_54), .gate(nT3));
  Transistor #(.\type ("n")) transistor_304 (.in(1'b0), .out(_54), .gate(or_1_out));
  Transistor #(.\type ("n")) transistor_305 (.in(1'b0), .out(_54), .gate(IR7));
  Transistor #(.\type ("n")) transistor_306 (.in(1'b0), .out(_54), .gate(IR4));
  Transistor #(.\type ("n")) transistor_307 (.in(1'b0), .out(_54), .gate(not_5_out));
  Transistor #(.\type ("n")) transistor_308 (.in(1'b0), .out(_54), .gate(not_6_out));
  Transistor #(.\type ("n")) transistor_309 (.in(1'b0), .out(_54), .gate(not_7_out));
  Pull_Resistor #(.pull(1)) pull_resistor_56 (.node(_55));
  Pull_Resistor #(.pull(1)) pull_resistor_57 (.node(_56));
  Transistor #(.\type ("n")) transistor_310 (.in(1'b0), .out(_56), .gate(nT5));
  Transistor #(.\type ("n")) transistor_311 (.in(1'b0), .out(_55), .gate(not_1_out));
  Transistor #(.\type ("n")) transistor_312 (.in(1'b0), .out(_56), .gate(or_1_out));
  Transistor #(.\type ("n")) transistor_313 (.in(1'b0), .out(_55), .gate(IR7));
  Transistor #(.\type ("n")) transistor_314 (.in(1'b0), .out(_56), .gate(IR7));
  Transistor #(.\type ("n")) transistor_315 (.in(1'b0), .out(_56), .gate(IR4));
  Transistor #(.\type ("n")) transistor_316 (.in(1'b0), .out(_56), .gate(IR3));
  Transistor #(.\type ("n")) transistor_317 (.in(1'b0), .out(_56), .gate(IR2));
  Transistor #(.\type ("n")) transistor_318 (.in(1'b0), .out(_55), .gate(IR6));
  Transistor #(.\type ("n")) transistor_319 (.in(1'b0), .out(_56), .gate(IR6));
  Transistor #(.\type ("n")) transistor_320 (.in(1'b0), .out(_56), .gate(not_8_out));
  Pull_Resistor #(.pull(1)) pull_resistor_58 (.node(_57));
  Transistor #(.\type ("n")) transistor_321 (.in(1'b0), .out(_57), .gate(nT2));
  Transistor #(.\type ("n")) transistor_322 (.in(1'b0), .out(_57), .gate(or_1_out));
  Transistor #(.\type ("n")) transistor_323 (.in(1'b0), .out(_57), .gate(IR7));
  Transistor #(.\type ("n")) transistor_324 (.in(1'b0), .out(_57), .gate(IR4));
  Transistor #(.\type ("n")) transistor_325 (.in(1'b0), .out(_57), .gate(IR2));
  Pull_Resistor #(.pull(1)) pull_resistor_59 (.node(_58));
  Transistor #(.\type ("n")) transistor_326 (.in(1'b0), .out(_58), .gate(or_1_out));
  Transistor #(.\type ("n")) transistor_327 (.in(1'b0), .out(_58), .gate(not_3_out));
  Transistor #(.\type ("n")) transistor_328 (.in(1'b0), .out(_58), .gate(not_4_out));
  Transistor #(.\type ("n")) transistor_329 (.in(1'b0), .out(_58), .gate(not_5_out));
  Transistor #(.\type ("n")) transistor_330 (.in(1'b0), .out(_58), .gate(IR2));
  Transistor #(.\type ("n")) transistor_331 (.in(1'b0), .out(_58), .gate(IR6));
  Transistor #(.\type ("n")) transistor_332 (.in(1'b0), .out(_58), .gate(IR5));
  Transistor #(.\type ("n")) transistor_333 (.in(1'b0), .out(_58), .gate(nT0X));
  Pull_Resistor #(.pull(1)) pull_resistor_60 (.node(_60));
  Pull_Resistor #(.pull(1)) pull_resistor_61 (.node(_59));
  Transistor #(.\type ("n")) transistor_334 (.in(1'b0), .out(_60), .gate(not_2_out));
  Transistor #(.\type ("n")) transistor_335 (.in(1'b0), .out(_59), .gate(not_2_out));
  Transistor #(.\type ("n")) transistor_336 (.in(1'b0), .out(_59), .gate(IR7));
  Transistor #(.\type ("n")) transistor_337 (.in(1'b0), .out(_60), .gate(not_7_out));
  Transistor #(.\type ("n")) transistor_338 (.in(1'b0), .out(_60), .gate(not_8_out));
  Transistor #(.\type ("n")) transistor_339 (.in(1'b0), .out(_60), .gate(nT1X));
  Transistor #(.\type ("n")) transistor_340 (.in(1'b0), .out(_59), .gate(nT1X));
  Pull_Resistor #(.pull(1)) pull_resistor_62 (.node(_61));
  Transistor #(.\type ("n")) transistor_341 (.in(1'b0), .out(_61), .gate(not_1_out));
  Transistor #(.\type ("n")) transistor_342 (.in(1'b0), .out(_61), .gate(IR7));
  Transistor #(.\type ("n")) transistor_343 (.in(1'b0), .out(_61), .gate(IR4));
  Transistor #(.\type ("n")) transistor_344 (.in(1'b0), .out(_61), .gate(IR2));
  Transistor #(.\type ("n")) transistor_345 (.in(1'b0), .out(_61), .gate(nT1X));
  Pull_Resistor #(.pull(1)) pull_resistor_63 (.node(_62));
  Transistor #(.\type ("n")) transistor_346 (.in(1'b0), .out(_62), .gate(not_1_out));
  Transistor #(.\type ("n")) transistor_347 (.in(1'b0), .out(_62), .gate(not_3_out));
  Transistor #(.\type ("n")) transistor_348 (.in(1'b0), .out(_62), .gate(IR4));
  Transistor #(.\type ("n")) transistor_349 (.in(1'b0), .out(_62), .gate(not_5_out));
  Transistor #(.\type ("n")) transistor_350 (.in(1'b0), .out(_62), .gate(IR2));
  Transistor #(.\type ("n")) transistor_351 (.in(1'b0), .out(_62), .gate(IR6));
  Transistor #(.\type ("n")) transistor_352 (.in(1'b0), .out(_62), .gate(IR5));
  Transistor #(.\type ("n")) transistor_353 (.in(1'b0), .out(_62), .gate(nT0X));
  Pull_Resistor #(.pull(1)) pull_resistor_64 (.node(_64));
  Pull_Resistor #(.pull(1)) pull_resistor_65 (.node(_63));
  Transistor #(.\type ("n")) transistor_354 (.in(1'b0), .out(_63), .gate(or_1_out));
  Transistor #(.\type ("n")) transistor_355 (.in(1'b0), .out(_64), .gate(not_2_out));
  Transistor #(.\type ("n")) transistor_356 (.in(1'b0), .out(_63), .gate(IR7));
  Transistor #(.\type ("n")) transistor_357 (.in(1'b0), .out(_64), .gate(not_3_out));
  Transistor #(.\type ("n")) transistor_358 (.in(1'b0), .out(_63), .gate(IR4));
  Transistor #(.\type ("n")) transistor_359 (.in(1'b0), .out(_63), .gate(not_5_out));
  Transistor #(.\type ("n")) transistor_360 (.in(1'b0), .out(_63), .gate(IR2));
  Transistor #(.\type ("n")) transistor_361 (.in(1'b0), .out(_64), .gate(IR6));
  Transistor #(.\type ("n")) transistor_362 (.in(1'b0), .out(_63), .gate(not_7_out));
  Transistor #(.\type ("n")) transistor_363 (.in(1'b0), .out(_64), .gate(not_8_out));
  Transistor #(.\type ("n")) transistor_364 (.in(1'b0), .out(_63), .gate(not_8_out));
  Transistor #(.\type ("n")) transistor_365 (.in(1'b0), .out(_63), .gate(nT0X));
  Transistor #(.\type ("n")) transistor_366 (.in(1'b0), .out(_64), .gate(nT0X));
  Pull_Resistor #(.pull(1)) pull_resistor_66 (.node(_65));
  Transistor #(.\type ("n")) transistor_367 (.in(1'b0), .out(_65), .gate(not_2_out));
  Transistor #(.\type ("n")) transistor_368 (.in(1'b0), .out(_65), .gate(nT0X));
  Pull_Resistor #(.pull(1)) pull_resistor_67 (.node(_66));
  Transistor #(.\type ("n")) transistor_369 (.in(1'b0), .out(_66), .gate(or_1_out));
  Transistor #(.\type ("n")) transistor_370 (.in(1'b0), .out(_66), .gate(not_3_out));
  Transistor #(.\type ("n")) transistor_371 (.in(1'b0), .out(_66), .gate(IR4));
  Transistor #(.\type ("n")) transistor_372 (.in(1'b0), .out(_66), .gate(not_5_out));
  Transistor #(.\type ("n")) transistor_373 (.in(1'b0), .out(_66), .gate(IR2));
  Transistor #(.\type ("n")) transistor_374 (.in(1'b0), .out(_66), .gate(IR6));
  Transistor #(.\type ("n")) transistor_375 (.in(1'b0), .out(_66), .gate(not_8_out));
  Transistor #(.\type ("n")) transistor_376 (.in(1'b0), .out(_66), .gate(nT0X));
  Pull_Resistor #(.pull(1)) pull_resistor_68 (.node(_67));
  Pull_Resistor #(.pull(1)) pull_resistor_69 (.node(_68));
  Transistor #(.\type ("n")) transistor_377 (.in(1'b0), .out(_67), .gate(not_1_out));
  Transistor #(.\type ("n")) transistor_378 (.in(1'b0), .out(_68), .gate(not_1_out));
  Transistor #(.\type ("n")) transistor_379 (.in(1'b0), .out(_67), .gate(IR7));
  Transistor #(.\type ("n")) transistor_380 (.in(1'b0), .out(_68), .gate(not_3_out));
  Transistor #(.\type ("n")) transistor_381 (.in(1'b0), .out(_68), .gate(IR4));
  Transistor #(.\type ("n")) transistor_382 (.in(1'b0), .out(_67), .gate(IR4));
  Transistor #(.\type ("n")) transistor_383 (.in(1'b0), .out(_67), .gate(not_5_out));
  Transistor #(.\type ("n")) transistor_384 (.in(1'b0), .out(_68), .gate(not_5_out));
  Transistor #(.\type ("n")) transistor_385 (.in(1'b0), .out(_68), .gate(IR2));
  Transistor #(.\type ("n")) transistor_386 (.in(1'b0), .out(_67), .gate(IR2));
  Transistor #(.\type ("n")) transistor_387 (.in(1'b0), .out(_68), .gate(IR6));
  Transistor #(.\type ("n")) transistor_388 (.in(1'b0), .out(_68), .gate(not_8_out));
  Transistor #(.\type ("n")) transistor_389 (.in(1'b0), .out(_67), .gate(nT0X));
  Transistor #(.\type ("n")) transistor_390 (.in(1'b0), .out(_68), .gate(nT0X));
  Pull_Resistor #(.pull(1)) pull_resistor_70 (.node(_69));
  Transistor #(.\type ("n")) transistor_391 (.in(1'b0), .out(_69), .gate(or_1_out));
  Transistor #(.\type ("n")) transistor_392 (.in(1'b0), .out(_69), .gate(IR7));
  Transistor #(.\type ("n")) transistor_393 (.in(1'b0), .out(_69), .gate(IR4));
  Transistor #(.\type ("n")) transistor_394 (.in(1'b0), .out(_69), .gate(not_6_out));
  Transistor #(.\type ("n")) transistor_395 (.in(1'b0), .out(_69), .gate(IR6));
  Transistor #(.\type ("n")) transistor_396 (.in(1'b0), .out(_69), .gate(not_8_out));
  Transistor #(.\type ("n")) transistor_397 (.in(1'b0), .out(_69), .gate(nT0X));
  Pull_Resistor #(.pull(1)) pull_resistor_71 (.node(_70));
  Transistor #(.\type ("n")) transistor_398 (.in(1'b0), .out(_70), .gate(not_2_out));
  Transistor #(.\type ("n")) transistor_399 (.in(1'b0), .out(_70), .gate(IR7));
  Transistor #(.\type ("n")) transistor_400 (.in(1'b0), .out(_70), .gate(IR6));
  Transistor #(.\type ("n")) transistor_401 (.in(1'b0), .out(_70), .gate(not_8_out));
  Transistor #(.\type ("n")) transistor_402 (.in(1'b0), .out(_70), .gate(nT0X));
  Pull_Resistor #(.pull(1)) pull_resistor_72 (.node(_71));
  Pull_Resistor #(.pull(1)) pull_resistor_73 (.node(_72));
  Transistor #(.\type ("n")) transistor_403 (.in(1'b0), .out(_72), .gate(nT5));
  Transistor #(.\type ("n")) transistor_404 (.in(1'b0), .out(_71), .gate(nT4));
  Transistor #(.\type ("n")) transistor_405 (.in(1'b0), .out(_72), .gate(not_2_out));
  Transistor #(.\type ("n")) transistor_406 (.in(1'b0), .out(_71), .gate(not_4_out));
  Transistor #(.\type ("n")) transistor_407 (.in(1'b0), .out(_72), .gate(not_4_out));
  Transistor #(.\type ("n")) transistor_408 (.in(1'b0), .out(_72), .gate(IR3));
  Transistor #(.\type ("n")) transistor_409 (.in(1'b0), .out(_71), .gate(not_5_out));
  Transistor #(.\type ("n")) transistor_410 (.in(1'b0), .out(_72), .gate(IR2));
  Pull_Resistor #(.pull(1)) pull_resistor_74 (.node(_73));
  Transistor #(.\type ("n")) transistor_411 (.in(1'b0), .out(_73), .gate(or_1_out));
  Transistor #(.\type ("n")) transistor_412 (.in(1'b0), .out(_73), .gate(not_4_out));
  Transistor #(.\type ("n")) transistor_413 (.in(1'b0), .out(_73), .gate(IR3));
  Transistor #(.\type ("n")) transistor_414 (.in(1'b0), .out(_73), .gate(IR2));
  Transistor #(.\type ("n")) transistor_415 (.in(1'b0), .out(_73), .gate(nT0X));
  Pull_Resistor #(.pull(1)) pull_resistor_75 (.node(_74));
  Pull_Resistor #(.pull(1)) pull_resistor_76 (.node(_75));
  Transistor #(.\type ("n")) transistor_416 (.in(1'b0), .out(_74), .gate(nT2));
  Transistor #(.\type ("n")) transistor_417 (.in(1'b0), .out(_75), .gate(not_1_out));
  Transistor #(.\type ("n")) transistor_418 (.in(1'b0), .out(_74), .gate(or_1_out));
  Transistor #(.\type ("n")) transistor_419 (.in(1'b0), .out(_74), .gate(IR7));
  Transistor #(.\type ("n")) transistor_420 (.in(1'b0), .out(_75), .gate(IR7));
  Transistor #(.\type ("n")) transistor_421 (.in(1'b0), .out(_74), .gate(IR4));
  Transistor #(.\type ("n")) transistor_422 (.in(1'b0), .out(_75), .gate(IR4));
  Transistor #(.\type ("n")) transistor_423 (.in(1'b0), .out(_74), .gate(not_5_out));
  Transistor #(.\type ("n")) transistor_424 (.in(1'b0), .out(_75), .gate(not_5_out));
  Transistor #(.\type ("n")) transistor_425 (.in(1'b0), .out(_75), .gate(IR2));
  Transistor #(.\type ("n")) transistor_426 (.in(1'b0), .out(_74), .gate(IR2));
  Transistor #(.\type ("n")) transistor_427 (.in(1'b0), .out(_75), .gate(not_7_out));
  Transistor #(.\type ("n")) transistor_428 (.in(1'b0), .out(_74), .gate(not_7_out));
  Transistor #(.\type ("n")) transistor_429 (.in(1'b0), .out(_74), .gate(IR5));
  Transistor #(.\type ("n")) transistor_430 (.in(1'b0), .out(_75), .gate(nT0X));
  Pull_Resistor #(.pull(1)) pull_resistor_77 (.node(_76));
  Transistor #(.\type ("n")) transistor_431 (.in(1'b0), .out(_76), .gate(not_1_out));
  Transistor #(.\type ("n")) transistor_432 (.in(1'b0), .out(_76), .gate(IR7));
  Transistor #(.\type ("n")) transistor_433 (.in(1'b0), .out(_76), .gate(not_7_out));
  Pull_Resistor #(.pull(1)) pull_resistor_78 (.node(_77));
  Transistor #(.\type ("n")) transistor_434 (.in(1'b0), .out(_77), .gate(nT2));
  Transistor #(.\type ("n")) transistor_435 (.in(1'b0), .out(_77), .gate(or_1_out));
  Transistor #(.\type ("n")) transistor_436 (.in(1'b0), .out(_77), .gate(IR7));
  Transistor #(.\type ("n")) transistor_437 (.in(1'b0), .out(_77), .gate(IR4));
  Transistor #(.\type ("n")) transistor_438 (.in(1'b0), .out(_77), .gate(IR3));
  Transistor #(.\type ("n")) transistor_439 (.in(1'b0), .out(_77), .gate(IR2));
  Transistor #(.\type ("n")) transistor_440 (.in(1'b0), .out(_77), .gate(IR6));
  Transistor #(.\type ("n")) transistor_441 (.in(1'b0), .out(_77), .gate(IR5));
  Pull_Resistor #(.pull(1)) pull_resistor_79 (.node(_78));
  Pull_Resistor #(.pull(1)) pull_resistor_80 (.node(_79));
  Transistor #(.\type ("n")) transistor_442 (.in(1'b0), .out(_78), .gate(nT3));
  Transistor #(.\type ("n")) transistor_443 (.in(1'b0), .out(_78), .gate(or_1_out));
  Transistor #(.\type ("n")) transistor_444 (.in(1'b0), .out(_79), .gate(not_2_out));
  Transistor #(.\type ("n")) transistor_445 (.in(1'b0), .out(_78), .gate(IR7));
  Transistor #(.\type ("n")) transistor_446 (.in(1'b0), .out(_79), .gate(not_3_out));
  Transistor #(.\type ("n")) transistor_447 (.in(1'b0), .out(_78), .gate(IR4));
  Transistor #(.\type ("n")) transistor_448 (.in(1'b0), .out(_78), .gate(IR3));
  Transistor #(.\type ("n")) transistor_449 (.in(1'b0), .out(_78), .gate(IR2));
  Transistor #(.\type ("n")) transistor_450 (.in(1'b0), .out(_78), .gate(IR6));
  Transistor #(.\type ("n")) transistor_451 (.in(1'b0), .out(_79), .gate(IR6));
  Transistor #(.\type ("n")) transistor_452 (.in(1'b0), .out(_79), .gate(IR5));
  Transistor #(.\type ("n")) transistor_453 (.in(1'b0), .out(_78), .gate(not_8_out));
  Pull_Resistor #(.pull(1)) pull_resistor_81 (.node(_80));
  Transistor #(.\type ("n")) transistor_454 (.in(1'b0), .out(_80), .gate(nT2));
  Transistor #(.\type ("n")) transistor_455 (.in(1'b0), .out(_80), .gate(or_1_out));
  Transistor #(.\type ("n")) transistor_456 (.in(1'b0), .out(_80), .gate(not_4_out));
  Transistor #(.\type ("n")) transistor_457 (.in(1'b0), .out(_80), .gate(IR3));
  Transistor #(.\type ("n")) transistor_458 (.in(1'b0), .out(_80), .gate(IR2));
  Pull_Resistor #(.pull(1)) pull_resistor_82 (.node(_81));
  Transistor #(.\type ("n")) transistor_459 (.in(1'b0), .out(_81), .gate(nT2));
  Transistor #(.\type ("n")) transistor_460 (.in(1'b0), .out(_81), .gate(IR3));
  Transistor #(.\type ("n")) transistor_461 (.in(1'b0), .out(_81), .gate(not_6_out));
  Pull_Resistor #(.pull(1)) pull_resistor_83 (.node(_83));
  Pull_Resistor #(.pull(1)) pull_resistor_84 (.node(_82));
  Transistor #(.\type ("n")) transistor_462 (.in(1'b0), .out(_83), .gate(nT2));
  Transistor #(.\type ("n")) transistor_463 (.in(1'b0), .out(_82), .gate(nT2));
  Transistor #(.\type ("n")) transistor_464 (.in(1'b0), .out(_82), .gate(not_2_out));
  Transistor #(.\type ("n")) transistor_465 (.in(1'b0), .out(_82), .gate(IR3));
  Transistor #(.\type ("n")) transistor_466 (.in(1'b0), .out(_83), .gate(not_5_out));
  Transistor #(.\type ("n")) transistor_467 (.in(1'b0), .out(_82), .gate(IR2));
  Pull_Resistor #(.pull(1)) pull_resistor_85 (.node(_84));
  Transistor #(.\type ("n")) transistor_468 (.in(1'b0), .out(_84), .gate(nT5));
  Transistor #(.\type ("n")) transistor_469 (.in(1'b0), .out(_84), .gate(or_1_out));
  Transistor #(.\type ("n")) transistor_470 (.in(1'b0), .out(_84), .gate(IR7));
  Transistor #(.\type ("n")) transistor_471 (.in(1'b0), .out(_84), .gate(IR4));
  Transistor #(.\type ("n")) transistor_472 (.in(1'b0), .out(_84), .gate(IR3));
  Transistor #(.\type ("n")) transistor_473 (.in(1'b0), .out(_84), .gate(IR2));
  Transistor #(.\type ("n")) transistor_474 (.in(1'b0), .out(_84), .gate(not_7_out));
  Transistor #(.\type ("n")) transistor_475 (.in(1'b0), .out(_84), .gate(not_8_out));
  Pull_Resistor #(.pull(1)) pull_resistor_86 (.node(_85));
  Transistor #(.\type ("n")) transistor_476 (.in(1'b0), .out(_85), .gate(nT4));
  Pull_Resistor #(.pull(1)) pull_resistor_87 (.node(_87));
  Pull_Resistor #(.pull(1)) pull_resistor_88 (.node(_86));
  Transistor #(.\type ("n")) transistor_477 (.in(1'b0), .out(_86), .gate(nT3));
  Transistor #(.\type ("n")) transistor_478 (.in(1'b0), .out(_87), .gate(or_1_out));
  Transistor #(.\type ("n")) transistor_479 (.in(1'b0), .out(_87), .gate(IR7));
  Transistor #(.\type ("n")) transistor_480 (.in(1'b0), .out(_87), .gate(IR4));
  Transistor #(.\type ("n")) transistor_481 (.in(1'b0), .out(_87), .gate(IR3));
  Transistor #(.\type ("n")) transistor_482 (.in(1'b0), .out(_87), .gate(IR2));
  Transistor #(.\type ("n")) transistor_483 (.in(1'b0), .out(_87), .gate(IR5));
  Transistor #(.\type ("n")) transistor_484 (.in(1'b0), .out(_87), .gate(nT0X));
  Pull_Resistor #(.pull(1)) pull_resistor_89 (.node(_88));
  Transistor #(.\type ("n")) transistor_485 (.in(1'b0), .out(_88), .gate(or_1_out));
  Transistor #(.\type ("n")) transistor_486 (.in(1'b0), .out(_88), .gate(IR7));
  Transistor #(.\type ("n")) transistor_487 (.in(1'b0), .out(_88), .gate(IR4));
  Transistor #(.\type ("n")) transistor_488 (.in(1'b0), .out(_88), .gate(not_5_out));
  Transistor #(.\type ("n")) transistor_489 (.in(1'b0), .out(_88), .gate(not_6_out));
  Transistor #(.\type ("n")) transistor_490 (.in(1'b0), .out(_88), .gate(not_7_out));
  Transistor #(.\type ("n")) transistor_491 (.in(1'b0), .out(_88), .gate(nT0X));
  Pull_Resistor #(.pull(1)) pull_resistor_90 (.node(_89));
  Transistor #(.\type ("n")) transistor_492 (.in(1'b0), .out(_89), .gate(nT5));
  Transistor #(.\type ("n")) transistor_493 (.in(1'b0), .out(_89), .gate(not_2_out));
  Transistor #(.\type ("n")) transistor_494 (.in(1'b0), .out(_89), .gate(IR4));
  Transistor #(.\type ("n")) transistor_495 (.in(1'b0), .out(_89), .gate(IR3));
  Transistor #(.\type ("n")) transistor_496 (.in(1'b0), .out(_89), .gate(IR2));
  Pull_Resistor #(.pull(1)) pull_resistor_91 (.node(_90));
  Transistor #(.\type ("n")) transistor_497 (.in(1'b0), .out(_90), .gate(nT3));
  Transistor #(.\type ("n")) transistor_498 (.in(1'b0), .out(_90), .gate(not_5_out));
  Pull_Resistor #(.pull(1)) pull_resistor_92 (.node(_91));
  Transistor #(.\type ("n")) transistor_499 (.in(1'b0), .out(_91), .gate(nT4));
  Transistor #(.\type ("n")) transistor_500 (.in(1'b0), .out(_91), .gate(not_2_out));
  Transistor #(.\type ("n")) transistor_501 (.in(1'b0), .out(_91), .gate(not_4_out));
  Transistor #(.\type ("n")) transistor_502 (.in(1'b0), .out(_91), .gate(IR3));
  Transistor #(.\type ("n")) transistor_503 (.in(1'b0), .out(_91), .gate(IR2));
  Pull_Resistor #(.pull(1)) pull_resistor_93 (.node(_92));
  Transistor #(.\type ("n")) transistor_504 (.in(1'b0), .out(_92), .gate(nT3));
  Transistor #(.\type ("n")) transistor_505 (.in(1'b0), .out(_92), .gate(not_4_out));
  Transistor #(.\type ("n")) transistor_506 (.in(1'b0), .out(_92), .gate(not_5_out));
  Pull_Resistor #(.pull(1)) pull_resistor_94 (.node(_93));
  Pull_Resistor #(.pull(1)) pull_resistor_95 (.node(_94));
  Transistor #(.\type ("n")) transistor_507 (.in(1'b0), .out(_93), .gate(nT3));
  Transistor #(.\type ("n")) transistor_508 (.in(1'b0), .out(_93), .gate(or_1_out));
  Transistor #(.\type ("n")) transistor_509 (.in(1'b0), .out(_94), .gate(or_1_out));
  Transistor #(.\type ("n")) transistor_510 (.in(1'b0), .out(_94), .gate(IR7));
  Transistor #(.\type ("n")) transistor_511 (.in(1'b0), .out(_94), .gate(IR4));
  Transistor #(.\type ("n")) transistor_512 (.in(1'b0), .out(_93), .gate(not_4_out));
  Transistor #(.\type ("n")) transistor_513 (.in(1'b0), .out(_93), .gate(IR3));
  Transistor #(.\type ("n")) transistor_514 (.in(1'b0), .out(_94), .gate(IR3));
  Transistor #(.\type ("n")) transistor_515 (.in(1'b0), .out(_94), .gate(IR2));
  Transistor #(.\type ("n")) transistor_516 (.in(1'b0), .out(_93), .gate(IR2));
  Transistor #(.\type ("n")) transistor_517 (.in(1'b0), .out(_94), .gate(IR5));
  Pull_Resistor #(.pull(1)) pull_resistor_96 (.node(_95));
  Transistor #(.\type ("n")) transistor_518 (.in(1'b0), .out(_95), .gate(or_1_out));
  Transistor #(.\type ("n")) transistor_519 (.in(1'b0), .out(_95), .gate(IR7));
  Transistor #(.\type ("n")) transistor_520 (.in(1'b0), .out(_95), .gate(IR4));
  Transistor #(.\type ("n")) transistor_521 (.in(1'b0), .out(_95), .gate(IR3));
  Transistor #(.\type ("n")) transistor_522 (.in(1'b0), .out(_95), .gate(IR2));
  Transistor #(.\type ("n")) transistor_523 (.in(1'b0), .out(_95), .gate(IR6));
  Transistor #(.\type ("n")) transistor_524 (.in(1'b0), .out(_95), .gate(not_8_out));
  Pull_Resistor #(.pull(1)) pull_resistor_97 (.node(_96));
  Transistor #(.\type ("n")) transistor_525 (.in(1'b0), .out(_96), .gate(or_1_out));
  Transistor #(.\type ("n")) transistor_526 (.in(1'b0), .out(_96), .gate(IR7));
  Transistor #(.\type ("n")) transistor_527 (.in(1'b0), .out(_96), .gate(IR4));
  Transistor #(.\type ("n")) transistor_528 (.in(1'b0), .out(_96), .gate(not_5_out));
  Transistor #(.\type ("n")) transistor_529 (.in(1'b0), .out(_96), .gate(not_6_out));
  Transistor #(.\type ("n")) transistor_530 (.in(1'b0), .out(_96), .gate(not_7_out));
  Pull_Resistor #(.pull(1)) pull_resistor_98 (.node(_97));
  Transistor #(.\type ("n")) transistor_531 (.in(1'b0), .out(_97), .gate(not_3_out));
  Transistor #(.\type ("n")) transistor_532 (.in(1'b0), .out(_97), .gate(IR6));
  Transistor #(.\type ("n")) transistor_533 (.in(1'b0), .out(_97), .gate(IR5));
  Pull_Resistor #(.pull(1)) pull_resistor_99 (.node(_98));
  Transistor #(.\type ("n")) transistor_534 (.in(1'b0), .out(_98), .gate(nT4));
  Transistor #(.\type ("n")) transistor_535 (.in(1'b0), .out(_98), .gate(or_1_out));
  Transistor #(.\type ("n")) transistor_536 (.in(1'b0), .out(_98), .gate(IR7));
  Transistor #(.\type ("n")) transistor_537 (.in(1'b0), .out(_98), .gate(IR4));
  Transistor #(.\type ("n")) transistor_538 (.in(1'b0), .out(_98), .gate(IR3));
  Transistor #(.\type ("n")) transistor_539 (.in(1'b0), .out(_98), .gate(IR2));
  Transistor #(.\type ("n")) transistor_540 (.in(1'b0), .out(_98), .gate(IR6));
  Transistor #(.\type ("n")) transistor_541 (.in(1'b0), .out(_98), .gate(IR5));
  Pull_Resistor #(.pull(1)) pull_resistor_100 (.node(_100));
  Pull_Resistor #(.pull(1)) pull_resistor_101 (.node(_99));
  Transistor #(.\type ("n")) transistor_542 (.in(1'b0), .out(_100), .gate(nT2));
  Transistor #(.\type ("n")) transistor_543 (.in(1'b0), .out(_99), .gate(nT2));
  Transistor #(.\type ("n")) transistor_544 (.in(1'b0), .out(_100), .gate(or_1_out));
  Transistor #(.\type ("n")) transistor_545 (.in(1'b0), .out(_99), .gate(or_1_out));
  Transistor #(.\type ("n")) transistor_546 (.in(1'b0), .out(_100), .gate(IR7));
  Transistor #(.\type ("n")) transistor_547 (.in(1'b0), .out(_99), .gate(IR7));
  Transistor #(.\type ("n")) transistor_548 (.in(1'b0), .out(_99), .gate(IR4));
  Transistor #(.\type ("n")) transistor_549 (.in(1'b0), .out(_100), .gate(IR4));
  Transistor #(.\type ("n")) transistor_550 (.in(1'b0), .out(_100), .gate(not_5_out));
  Transistor #(.\type ("n")) transistor_551 (.in(1'b0), .out(_99), .gate(not_5_out));
  Transistor #(.\type ("n")) transistor_552 (.in(1'b0), .out(_99), .gate(IR2));
  Transistor #(.\type ("n")) transistor_553 (.in(1'b0), .out(_100), .gate(IR2));
  Transistor #(.\type ("n")) transistor_554 (.in(1'b0), .out(_99), .gate(IR6));
  Transistor #(.\type ("n")) transistor_555 (.in(1'b0), .out(_100), .gate(IR5));
  Transistor #(.\type ("n")) transistor_556 (.in(1'b0), .out(_99), .gate(IR5));
  Pull_Resistor #(.pull(1)) pull_resistor_102 (.node(_101));
  Transistor #(.\type ("n")) transistor_557 (.in(1'b0), .out(_101), .gate(nT4));
  Transistor #(.\type ("n")) transistor_558 (.in(1'b0), .out(_101), .gate(or_1_out));
  Transistor #(.\type ("n")) transistor_559 (.in(1'b0), .out(_101), .gate(IR7));
  Transistor #(.\type ("n")) transistor_560 (.in(1'b0), .out(_101), .gate(IR4));
  Transistor #(.\type ("n")) transistor_561 (.in(1'b0), .out(_101), .gate(not_5_out));
  Transistor #(.\type ("n")) transistor_562 (.in(1'b0), .out(_101), .gate(not_6_out));
  Transistor #(.\type ("n")) transistor_563 (.in(1'b0), .out(_101), .gate(not_7_out));
  Pull_Resistor #(.pull(1)) pull_resistor_103 (.node(_102));
  Transistor #(.\type ("n")) transistor_564 (.in(1'b0), .out(_102), .gate(nT5));
  Transistor #(.\type ("n")) transistor_565 (.in(1'b0), .out(_102), .gate(or_1_out));
  Transistor #(.\type ("n")) transistor_566 (.in(1'b0), .out(_102), .gate(IR7));
  Transistor #(.\type ("n")) transistor_567 (.in(1'b0), .out(_102), .gate(IR4));
  Transistor #(.\type ("n")) transistor_568 (.in(1'b0), .out(_102), .gate(IR3));
  Transistor #(.\type ("n")) transistor_569 (.in(1'b0), .out(_102), .gate(IR2));
  Transistor #(.\type ("n")) transistor_570 (.in(1'b0), .out(_102), .gate(not_7_out));
  Pull_Resistor #(.pull(1)) pull_resistor_104 (.node(_103));
  Transistor #(.\type ("n")) transistor_571 (.in(1'b0), .out(_103), .gate(nT5));
  Transistor #(.\type ("n")) transistor_572 (.in(1'b0), .out(_103), .gate(or_1_out));
  Transistor #(.\type ("n")) transistor_573 (.in(1'b0), .out(_103), .gate(IR7));
  Transistor #(.\type ("n")) transistor_574 (.in(1'b0), .out(_103), .gate(IR4));
  Transistor #(.\type ("n")) transistor_575 (.in(1'b0), .out(_103), .gate(IR3));
  Transistor #(.\type ("n")) transistor_576 (.in(1'b0), .out(_103), .gate(IR2));
  Transistor #(.\type ("n")) transistor_577 (.in(1'b0), .out(_103), .gate(IR6));
  Transistor #(.\type ("n")) transistor_578 (.in(1'b0), .out(_103), .gate(not_8_out));
  Pull_Resistor #(.pull(1)) pull_resistor_105 (.node(_105));
  Pull_Resistor #(.pull(1)) pull_resistor_106 (.node(_104));
  Transistor #(.\type ("n")) transistor_579 (.in(1'b0), .out(_105), .gate(nT3));
  Transistor #(.\type ("n")) transistor_580 (.in(1'b0), .out(_104), .gate(nT2));
  Transistor #(.\type ("n")) transistor_581 (.in(1'b0), .out(_104), .gate(or_1_out));
  Transistor #(.\type ("n")) transistor_582 (.in(1'b0), .out(_105), .gate(or_1_out));
  Transistor #(.\type ("n")) transistor_583 (.in(1'b0), .out(_105), .gate(IR7));
  Transistor #(.\type ("n")) transistor_584 (.in(1'b0), .out(_104), .gate(IR7));
  Transistor #(.\type ("n")) transistor_585 (.in(1'b0), .out(_105), .gate(IR4));
  Transistor #(.\type ("n")) transistor_586 (.in(1'b0), .out(_104), .gate(IR4));
  Transistor #(.\type ("n")) transistor_587 (.in(1'b0), .out(_105), .gate(not_5_out));
  Transistor #(.\type ("n")) transistor_588 (.in(1'b0), .out(_104), .gate(not_5_out));
  Transistor #(.\type ("n")) transistor_589 (.in(1'b0), .out(_105), .gate(IR2));
  Transistor #(.\type ("n")) transistor_590 (.in(1'b0), .out(_104), .gate(not_6_out));
  Transistor #(.\type ("n")) transistor_591 (.in(1'b0), .out(_104), .gate(not_7_out));
  Transistor #(.\type ("n")) transistor_592 (.in(1'b0), .out(_104), .gate(IR5));
  Transistor #(.\type ("n")) transistor_593 (.in(1'b0), .out(_105), .gate(not_8_out));
  Pull_Resistor #(.pull(1)) pull_resistor_107 (.node(_106));
  Transistor #(.\type ("n")) transistor_594 (.in(1'b0), .out(_106), .gate(not_1_out));
  Transistor #(.\type ("n")) transistor_595 (.in(1'b0), .out(_106), .gate(not_7_out));
  Pull_Resistor #(.pull(1)) pull_resistor_108 (.node(_107));
  Transistor #(.\type ("n")) transistor_596 (.in(1'b0), .out(_107), .gate(not_1_out));
  Transistor #(.\type ("n")) transistor_597 (.in(1'b0), .out(_107), .gate(IR7));
  Transistor #(.\type ("n")) transistor_598 (.in(1'b0), .out(_107), .gate(IR6));
  Pull_Resistor #(.pull(1)) pull_resistor_109 (.node(_108));
  Transistor #(.\type ("n")) transistor_599 (.in(1'b0), .out(_108), .gate(or_1_out));
  Transistor #(.\type ("n")) transistor_600 (.in(1'b0), .out(_108), .gate(IR7));
  Transistor #(.\type ("n")) transistor_601 (.in(1'b0), .out(_108), .gate(not_4_out));
  Transistor #(.\type ("n")) transistor_602 (.in(1'b0), .out(_108), .gate(IR2));
  Transistor #(.\type ("n")) transistor_603 (.in(1'b0), .out(_108), .gate(not_7_out));
  Transistor #(.\type ("n")) transistor_604 (.in(1'b0), .out(_108), .gate(nT0X));
  Pull_Resistor #(.pull(1)) pull_resistor_110 (.node(_109));
  Transistor #(.\type ("n")) transistor_605 (.in(1'b0), .out(_109), .gate(or_1_out));
  Transistor #(.\type ("n")) transistor_606 (.in(1'b0), .out(_109), .gate(IR7));
  Transistor #(.\type ("n")) transistor_607 (.in(1'b0), .out(_109), .gate(IR4));
  Transistor #(.\type ("n")) transistor_608 (.in(1'b0), .out(_109), .gate(not_6_out));
  Transistor #(.\type ("n")) transistor_609 (.in(1'b0), .out(_109), .gate(IR6));
  Transistor #(.\type ("n")) transistor_610 (.in(1'b0), .out(_109), .gate(not_8_out));
  Transistor #(.\type ("n")) transistor_611 (.in(1'b0), .out(_109), .gate(nT1X));
  Pull_Resistor #(.pull(1)) pull_resistor_111 (.node(_110));
  Pull_Resistor #(.pull(1)) pull_resistor_112 (.node(_111));
  Transistor #(.\type ("n")) transistor_612 (.in(1'b0), .out(_111), .gate(nT3));
  Transistor #(.\type ("n")) transistor_613 (.in(1'b0), .out(_110), .gate(or_1_out));
  Transistor #(.\type ("n")) transistor_614 (.in(1'b0), .out(_110), .gate(IR7));
  Transistor #(.\type ("n")) transistor_615 (.in(1'b0), .out(_111), .gate(not_4_out));
  Transistor #(.\type ("n")) transistor_616 (.in(1'b0), .out(_110), .gate(not_4_out));
  Transistor #(.\type ("n")) transistor_617 (.in(1'b0), .out(_111), .gate(IR3));
  Transistor #(.\type ("n")) transistor_618 (.in(1'b0), .out(_110), .gate(not_5_out));
  Transistor #(.\type ("n")) transistor_619 (.in(1'b0), .out(_110), .gate(IR2));
  Transistor #(.\type ("n")) transistor_620 (.in(1'b0), .out(_111), .gate(not_6_out));
  Transistor #(.\type ("n")) transistor_621 (.in(1'b0), .out(_110), .gate(IR6));
  Transistor #(.\type ("n")) transistor_622 (.in(1'b0), .out(_110), .gate(nT0X));
  Pull_Resistor #(.pull(1)) pull_resistor_113 (.node(_112));
  Transistor #(.\type ("n")) transistor_623 (.in(1'b0), .out(_112), .gate(not_2_out));
  Transistor #(.\type ("n")) transistor_624 (.in(1'b0), .out(_112), .gate(not_7_out));
  Transistor #(.\type ("n")) transistor_625 (.in(1'b0), .out(_112), .gate(not_8_out));
  Transistor #(.\type ("n")) transistor_626 (.in(1'b0), .out(_112), .gate(nT1X));
  Pull_Resistor #(.pull(1)) pull_resistor_114 (.node(_113));
  Transistor #(.\type ("n")) transistor_627 (.in(1'b0), .out(_113), .gate(or_1_out));
  Transistor #(.\type ("n")) transistor_628 (.in(1'b0), .out(_113), .gate(IR7));
  Transistor #(.\type ("n")) transistor_629 (.in(1'b0), .out(_113), .gate(IR4));
  Transistor #(.\type ("n")) transistor_630 (.in(1'b0), .out(_113), .gate(not_6_out));
  Transistor #(.\type ("n")) transistor_631 (.in(1'b0), .out(_113), .gate(IR6));
  Transistor #(.\type ("n")) transistor_632 (.in(1'b0), .out(_113), .gate(not_8_out));
  Transistor #(.\type ("n")) transistor_633 (.in(1'b0), .out(_113), .gate(nT0X));
  Pull_Resistor #(.pull(1)) pull_resistor_115 (.node(_115));
  Pull_Resistor #(.pull(1)) pull_resistor_116 (.node(_114));
  Transistor #(.\type ("n")) transistor_634 (.in(1'b0), .out(_115), .gate(nT4));
  Transistor #(.\type ("n")) transistor_635 (.in(1'b0), .out(_114), .gate(or_1_out));
  Transistor #(.\type ("n")) transistor_636 (.in(1'b0), .out(_115), .gate(or_1_out));
  Transistor #(.\type ("n")) transistor_637 (.in(1'b0), .out(_114), .gate(IR7));
  Transistor #(.\type ("n")) transistor_638 (.in(1'b0), .out(_115), .gate(IR7));
  Transistor #(.\type ("n")) transistor_639 (.in(1'b0), .out(_114), .gate(IR4));
  Transistor #(.\type ("n")) transistor_640 (.in(1'b0), .out(_115), .gate(IR4));
  Transistor #(.\type ("n")) transistor_641 (.in(1'b0), .out(_115), .gate(IR3));
  Transistor #(.\type ("n")) transistor_642 (.in(1'b0), .out(_114), .gate(not_5_out));
  Transistor #(.\type ("n")) transistor_643 (.in(1'b0), .out(_114), .gate(IR2));
  Transistor #(.\type ("n")) transistor_644 (.in(1'b0), .out(_115), .gate(IR2));
  Transistor #(.\type ("n")) transistor_645 (.in(1'b0), .out(_114), .gate(IR6));
  Transistor #(.\type ("n")) transistor_646 (.in(1'b0), .out(_115), .gate(not_7_out));
  Transistor #(.\type ("n")) transistor_647 (.in(1'b0), .out(_115), .gate(IR5));
  Transistor #(.\type ("n")) transistor_648 (.in(1'b0), .out(_114), .gate(not_8_out));
  Transistor #(.\type ("n")) transistor_649 (.in(1'b0), .out(_114), .gate(nT0X));
  Pull_Resistor #(.pull(1)) pull_resistor_117 (.node(_116));
  Transistor #(.\type ("n")) transistor_650 (.in(1'b0), .out(_116), .gate(not_2_out));
  Transistor #(.\type ("n")) transistor_651 (.in(1'b0), .out(_116), .gate(not_3_out));
  Transistor #(.\type ("n")) transistor_652 (.in(1'b0), .out(_116), .gate(not_7_out));
  Transistor #(.\type ("n")) transistor_653 (.in(1'b0), .out(_116), .gate(IR5));
  Transistor #(.\type ("n")) transistor_654 (.in(1'b0), .out(_116), .gate(nT1X));
  Pull_Resistor #(.pull(1)) pull_resistor_118 (.node(_117));
  Transistor #(.\type ("n")) transistor_655 (.in(1'b0), .out(_117), .gate(or_1_out));
  Transistor #(.\type ("n")) transistor_656 (.in(1'b0), .out(_117), .gate(not_3_out));
  Transistor #(.\type ("n")) transistor_657 (.in(1'b0), .out(_117), .gate(IR4));
  Transistor #(.\type ("n")) transistor_658 (.in(1'b0), .out(_117), .gate(not_5_out));
  Transistor #(.\type ("n")) transistor_659 (.in(1'b0), .out(_117), .gate(not_6_out));
  Transistor #(.\type ("n")) transistor_660 (.in(1'b0), .out(_117), .gate(not_7_out));
  Transistor #(.\type ("n")) transistor_661 (.in(1'b0), .out(_117), .gate(nT1X));
  Pull_Resistor #(.pull(1)) pull_resistor_119 (.node(_118));
  Pull_Resistor #(.pull(1)) pull_resistor_120 (.node(_119));
  Transistor #(.\type ("n")) transistor_662 (.in(1'b0), .out(_118), .gate(not_1_out));
  Transistor #(.\type ("n")) transistor_663 (.in(1'b0), .out(_119), .gate(or_1_out));
  Transistor #(.\type ("n")) transistor_664 (.in(1'b0), .out(_118), .gate(IR7));
  Transistor #(.\type ("n")) transistor_665 (.in(1'b0), .out(_119), .gate(not_3_out));
  Transistor #(.\type ("n")) transistor_666 (.in(1'b0), .out(_119), .gate(IR4));
  Transistor #(.\type ("n")) transistor_667 (.in(1'b0), .out(_118), .gate(IR4));
  Transistor #(.\type ("n")) transistor_668 (.in(1'b0), .out(_119), .gate(IR3));
  Transistor #(.\type ("n")) transistor_669 (.in(1'b0), .out(_118), .gate(not_5_out));
  Transistor #(.\type ("n")) transistor_670 (.in(1'b0), .out(_118), .gate(IR2));
  Transistor #(.\type ("n")) transistor_671 (.in(1'b0), .out(_118), .gate(IR6));
  Transistor #(.\type ("n")) transistor_672 (.in(1'b0), .out(_119), .gate(not_7_out));
  Transistor #(.\type ("n")) transistor_673 (.in(1'b0), .out(_118), .gate(nT1X));
  Transistor #(.\type ("n")) transistor_674 (.in(1'b0), .out(_119), .gate(nT1X));
  Pull_Resistor #(.pull(1)) pull_resistor_121 (.node(_120));
  Pull_Resistor #(.pull(1)) pull_resistor_122 (.node(_121));
  Transistor #(.\type ("n")) transistor_675 (.in(1'b0), .out(_120), .gate(or_1_out));
  Transistor #(.\type ("n")) transistor_676 (.in(1'b0), .out(_120), .gate(not_3_out));
  Transistor #(.\type ("n")) transistor_677 (.in(1'b0), .out(_120), .gate(not_4_out));
  Transistor #(.\type ("n")) transistor_678 (.in(1'b0), .out(_120), .gate(not_5_out));
  Transistor #(.\type ("n")) transistor_679 (.in(1'b0), .out(_120), .gate(IR2));
  Transistor #(.\type ("n")) transistor_680 (.in(1'b0), .out(_121), .gate(IR6));
  Transistor #(.\type ("n")) transistor_681 (.in(1'b0), .out(_120), .gate(not_7_out));
  Transistor #(.\type ("n")) transistor_682 (.in(1'b0), .out(_120), .gate(nT0X));
  Pull_Resistor #(.pull(1)) pull_resistor_123 (.node(_122));
  Transistor #(.\type ("n")) transistor_683 (.in(1'b0), .out(_122), .gate(nT3));
  Transistor #(.\type ("n")) transistor_684 (.in(1'b0), .out(_122), .gate(IR4));
  Transistor #(.\type ("n")) transistor_685 (.in(1'b0), .out(_122), .gate(not_5_out));
  Transistor #(.\type ("n")) transistor_686 (.in(1'b0), .out(_122), .gate(not_6_out));
  Pull_Resistor #(.pull(1)) pull_resistor_124 (.node(_123));
  Transistor #(.\type ("n")) transistor_687 (.in(1'b0), .out(_123), .gate(nT2));
  Transistor #(.\type ("n")) transistor_688 (.in(1'b0), .out(_123), .gate(IR4));
  Transistor #(.\type ("n")) transistor_689 (.in(1'b0), .out(_123), .gate(IR3));
  Transistor #(.\type ("n")) transistor_690 (.in(1'b0), .out(_123), .gate(not_6_out));
  Pull_Resistor #(.pull(1)) pull_resistor_125 (.node(_124));
  Pull_Resistor #(.pull(1)) pull_resistor_126 (.node(_125));
  Transistor #(.\type ("n")) transistor_691 (.in(1'b0), .out(_124), .gate(nT5));
  Transistor #(.\type ("n")) transistor_692 (.in(1'b0), .out(_125), .gate(nT4));
  Transistor #(.\type ("n")) transistor_693 (.in(1'b0), .out(_124), .gate(not_2_out));
  Transistor #(.\type ("n")) transistor_694 (.in(1'b0), .out(_125), .gate(not_4_out));
  Transistor #(.\type ("n")) transistor_695 (.in(1'b0), .out(_124), .gate(IR3));
  Transistor #(.\type ("n")) transistor_696 (.in(1'b0), .out(_125), .gate(not_5_out));
  Transistor #(.\type ("n")) transistor_697 (.in(1'b0), .out(_124), .gate(IR2));
  Pull_Resistor #(.pull(1)) pull_resistor_127 (.node(_126));
  Transistor #(.\type ("n")) transistor_698 (.in(1'b0), .out(_126), .gate(IR7));
  Pull_Resistor #(.pull(1)) pull_resistor_128 (.node(_127));
  Transistor #(.\type ("n")) transistor_699 (.in(1'b0), .out(_127), .gate(or_1_out));
  Transistor #(.\type ("n")) transistor_700 (.in(1'b0), .out(_127), .gate(not_3_out));
  Transistor #(.\type ("n")) transistor_701 (.in(1'b0), .out(_127), .gate(not_4_out));
  Transistor #(.\type ("n")) transistor_702 (.in(1'b0), .out(_127), .gate(not_5_out));
  Transistor #(.\type ("n")) transistor_703 (.in(1'b0), .out(_127), .gate(IR2));
  Transistor #(.\type ("n")) transistor_704 (.in(1'b0), .out(_127), .gate(IR6));
  Transistor #(.\type ("n")) transistor_705 (.in(1'b0), .out(_127), .gate(not_8_out));
  Pull_Resistor #(.pull(1)) pull_resistor_129 (.node(_129));
  Pull_Resistor #(.pull(1)) pull_resistor_130 (.node(_128));
  Transistor #(.\type ("n")) transistor_706 (.in(1'b0), .out(_128), .gate(IR0));
  Transistor #(.\type ("n")) transistor_707 (.in(1'b0), .out(_129), .gate(or_1_out));
  Transistor #(.\type ("n")) transistor_708 (.in(1'b0), .out(_129), .gate(IR7));
  Transistor #(.\type ("n")) transistor_709 (.in(1'b0), .out(_129), .gate(IR4));
  Transistor #(.\type ("n")) transistor_710 (.in(1'b0), .out(_129), .gate(not_5_out));
  Transistor #(.\type ("n")) transistor_711 (.in(1'b0), .out(_128), .gate(not_5_out));
  Transistor #(.\type ("n")) transistor_712 (.in(1'b0), .out(_129), .gate(IR2));
  Transistor #(.\type ("n")) transistor_713 (.in(1'b0), .out(_128), .gate(IR2));
endmodule

module PREDECODE (
  input  PHI0,
  input  _0_IR,
  input  D0,
  input  D1,
  input  D2,
  input  D3,
  input  D4,
  input  D5,
  input  D6,
  input  D7,
  output nIMPLIED,
  output nTWOCYCLE,
  output PD0,
  output PD1,
  output PD2,
  output PD3,
  output PD4,
  output PD5,
  output PD6,
  output PD7
);

  wire d_latch_1_out, d_latch_2_out, d_latch_3_out, d_latch_4_out, d_latch_5_out, d_latch_6_out,
       d_latch_7_out, d_latch_8_out, nand_1_out, nor_1_out, nor_2_out, nor_3_out, nor_4_out, not_1_out,
       not_2_out, not_3_out, not_4_out, not_5_out, or_1_out;

  not not_1 (not_1_out, _0_IR);
  D_LATCH d_latch_1 (.EN(PHI0), .in(D0), .out(d_latch_1_out));  // open: out_2
  D_LATCH d_latch_2 (.EN(PHI0), .in(D1), .out(d_latch_2_out));  // open: out_2
  D_LATCH d_latch_3 (.EN(PHI0), .in(D2), .out(d_latch_3_out));  // open: out_2
  D_LATCH d_latch_4 (.EN(PHI0), .in(D3), .out(d_latch_4_out));  // open: out_2
  D_LATCH d_latch_5 (.EN(PHI0), .in(D4), .out(d_latch_5_out));  // open: out_2
  D_LATCH d_latch_6 (.EN(PHI0), .in(D5), .out(d_latch_6_out));  // open: out_2
  D_LATCH d_latch_7 (.EN(PHI0), .in(D6), .out(d_latch_7_out));  // open: out_2
  D_LATCH d_latch_8 (.EN(PHI0), .in(D7), .out(d_latch_8_out));  // open: out_2
  and and_1 (PD0, d_latch_1_out, not_1_out);
  and and_2 (PD1, d_latch_2_out, not_1_out);
  and and_3 (PD2, d_latch_3_out, not_1_out);
  and and_4 (PD3, d_latch_4_out, not_1_out);
  and and_5 (PD4, d_latch_5_out, not_1_out);
  and and_6 (PD5, d_latch_6_out, not_1_out);
  and and_7 (PD6, d_latch_7_out, not_1_out);
  and and_8 (PD7, d_latch_8_out, not_1_out);
  not not_2 (not_2_out, PD3);
  nor nor_1 (nor_1_out, PD0, PD2, not_2_out);
  or or_1 (or_1_out, PD1, PD4, PD7);
  not not_3 (not_3_out, PD0);
  not not_4 (not_4_out, PD3);
  nor nor_2 (nor_2_out, not_3_out, PD2, not_4_out, PD4);
  not not_5 (not_5_out, PD7);
  nor nor_3 (nor_3_out, PD0, PD2, PD3, PD4, not_5_out);
  nand nand_1 (nand_1_out, nor_1_out, or_1_out);
  nor nor_4 (nor_4_out, nor_2_out, nor_3_out);
  not not_6 (nIMPLIED, nor_1_out);
  and and_9 (nTWOCYCLE, nand_1_out, nor_4_out);
endmodule

module IR (
  input  FETCH,
  input  PHI0,
  input  nPD0,
  input  nPD1,
  input  nPD2,
  input  nPD3,
  input  nPD4,
  input  nPD5,
  input  nPD6,
  input  nPD7,
  output IR0,
  output IR1,
  output IR2,
  output IR3,
  output IR4,
  output IR5,
  output IR6,
  output IR7
);

  wire and_1_out, not_1_out;

  not not_1 (not_1_out, PHI0);
  and and_1 (and_1_out, FETCH, not_1_out);
  D_LATCH d_latch_1 (.EN(and_1_out), .in(nPD0), .out_2(IR0));  // open: out
  D_LATCH d_latch_2 (.EN(and_1_out), .in(nPD1), .out_2(IR1));  // open: out
  D_LATCH d_latch_3 (.EN(and_1_out), .in(nPD2), .out_2(IR2));  // open: out
  D_LATCH d_latch_4 (.EN(and_1_out), .in(nPD3), .out_2(IR3));  // open: out
  D_LATCH d_latch_5 (.EN(and_1_out), .in(nPD4), .out_2(IR4));  // open: out
  D_LATCH d_latch_6 (.EN(and_1_out), .in(nPD5), .out_2(IR5));  // open: out
  D_LATCH d_latch_7 (.EN(and_1_out), .in(nPD6), .out_2(IR6));  // open: out
  D_LATCH d_latch_8 (.EN(and_1_out), .in(nPD7), .out_2(IR7));  // open: out
endmodule

module D_LATCH (
  input  EN,
  input  in,
  output out,
  output out_2
);

  D_Flip_Flop #(.trigger("high")) d_ff_1 (.clk(EN), .D(in), .Q(out), .Qn(out_2));  // open: preset, en, reset
endmodule

module Dispatch_test (
  input  nready,
  input  in_2,
  input  in_3,
  input  in_4,
  input  BR3,
  input  nTWOCYCLE,
  input  in_7,
  input  in_8,
  input  in_9,
  input  ACRL1,
  input  REST,
  input  in_12,
  input  RESP,
  input  BRK6E,
  input  in_15,
  output nT2,
  output nT3,
  output nT4,
  output nT5
);

  wire and_1_out, and_2_out, and_3_out, and_4_out, and_5_out, and_6_out, and_7_out, and_8_out,
       d_latch_1_out_2, d_latch_2_out_2, d_latch_3_out, d_latch_4_out, d_latch_5_out, d_latch_6_out,
       d_latch_7_out, d_latch_8_out_2, d_latch_9_out, d_latch_10_out, d_latch_11_out, d_latch_12_out,
       d_latch_12_out_2, d_latch_13_out_2, d_latch_14_out, d_latch_15_out, d_latch_16_out, d_latch_17_out_2,
       d_latch_18_out, d_latch_19_out, d_latch_20_out, d_latch_21_out, d_latch_22_out, d_latch_23_out,
       d_latch_24_out, d_latch_25_out, d_latch_26_out, multiplexer_1_out, nand_1_out, nand_2_out, nand_3_out,
       nand_4_out, nand_5_out, nand_6_out, nor_1_out, nor_2_out, nor_3_out, nor_4_out, nor_5_out, nor_6_out,
       nor_7_out, nor_8_out, nor_9_out, nor_10_out, nor_11_out, nor_12_out, nor_13_out, nor_14_out,
       nor_15_out, nor_16_out, nor_17_out, nor_18_out, not_1_out, not_2_out, not_3_out, not_4_out, not_5_out,
       not_6_out, not_7_out, not_8_out, not_9_out, not_10_out, not_11_out, not_12_out, not_13_out,
       not_14_out, not_15_out, not_16_out, not_17_out, not_18_out, not_19_out, not_20_out, not_21_out,
       not_22_out, not_23_out, not_24_out, not_25_out, or_1_out, or_2_out, or_3_out, or_4_out, PHI0_out,
       xnor_1_out;

  Clock PHI0 (.out(PHI0_out));
  not not_1 (not_1_out, PHI0_out);
  D_LATCH d_latch_1 (.EN(not_1_out), .in(nready), .out_2(d_latch_1_out_2));  // open: out
  D_LATCH d_latch_2 (.EN(PHI0_out), .in(d_latch_1_out_2), .out_2(d_latch_2_out_2));  // open: out
  not not_2 (not_2_out, PHI0_out);
  not not_3 (not_3_out, PHI0_out);
  not not_4 (not_4_out, PHI0_out);
  not not_5 (not_5_out, BR3);
  nor nor_1 (nor_1_out, not_5_out, d_latch_2_out_2);
  D_LATCH d_latch_3 (.EN(not_2_out), .in(nor_7_out), .out(d_latch_3_out));  // open: out_2
  D_LATCH d_latch_4 (.EN(not_3_out), .in(nTWOCYCLE), .out(d_latch_4_out));  // open: out_2
  D_LATCH d_latch_5 (.EN(not_4_out), .in(not_17_out), .out(d_latch_5_out));  // open: out_2
  not not_6 (not_6_out, d_latch_17_out_2);
  nand nand_1 (nand_1_out, in_7, in_8);
  not not_7 (not_7_out, not_12_out);
  D_LATCH d_latch_6 (.EN(PHI0_out), .in(nor_1_out), .out(d_latch_6_out));  // open: out_2
  nand nand_2 (nand_2_out, d_latch_3_out, d_latch_4_out);
  not not_8 (not_8_out, d_latch_5_out);
  Multiplexer multiplexer_1 (.in0(and_1_out), .in1(not_6_out), .out(multiplexer_1_out), .sel(nready));  // open: en
  and and_1 (and_1_out, nand_1_out, not_7_out);
  D_LATCH d_latch_7 (.EN(PHI0_out), .in(in_12), .out(d_latch_7_out));  // open: out_2
  nor nor_2 (nor_2_out, nready, in_15);
  and and_2 (and_2_out, nand_2_out, not_8_out);
  nor nor_3 (nor_3_out, nready, ACRL1, REST, d_latch_7_out);
  D_LATCH d_latch_8 (.EN(PHI0_out), .in(nor_4_out), .out_2(d_latch_8_out_2));  // open: out
  nor nor_4 (nor_4_out, RESP, nor_10_out, nor_2_out);
  xnor xnor_1 (xnor_1_out, in_3, in_4);
  nor nor_5 (nor_5_out, d_latch_11_out, d_latch_12_out);
  nor nor_6 (nor_6_out, d_latch_11_out, nready);
  nor nor_7 (nor_7_out, nor_3_out, d_latch_8_out_2);
  and and_3 (and_3_out, xnor_1_out, d_latch_6_out);
  nor nor_8 (nor_8_out, and_2_out, nor_5_out);
  D_LATCH d_latch_9 (.EN(PHI0_out), .in(multiplexer_1_out), .out(d_latch_9_out));  // open: out_2
  D_LATCH d_latch_10 (.EN(PHI0_out), .in(in_9), .out(d_latch_10_out));  // open: out_2
  not not_9 (not_9_out, BRK6E);
  nor nor_9 (nor_9_out, and_2_out, nor_5_out);
  D_LATCH d_latch_11 (.EN(PHI0_out), .in(nor_8_out), .out(d_latch_11_out));  // open: out_2
  D_LATCH d_latch_12 (.EN(not_10_out), .in(nor_6_out), .out(d_latch_12_out), .out_2(d_latch_12_out_2));
  not not_10 (not_10_out, PHI0_out);
  nor nor_10 (nor_10_out, d_latch_9_out, d_latch_10_out);
  not not_11 (not_11_out, PHI0_out);
  and and_4 (and_4_out, nor_7_out, not_9_out);
  not not_12 (not_12_out, nor_8_out);
  D_LATCH d_latch_13 (.EN(not_11_out), .in(and_4_out), .out_2(d_latch_13_out_2));  // open: out
  not not_13 (not_13_out, PHI0_out);
  not not_14 (not_14_out, nready);
  D_LATCH d_latch_14 (.EN(not_13_out), .in(not_14_out), .out(d_latch_14_out));  // open: out_2
  nor nor_11 (nor_11_out, in_2, d_latch_14_out, d_latch_16_out);
  nor nor_12 (nor_12_out, d_latch_15_out, and_3_out);
  nor nor_13 (nor_13_out, nready, nor_12_out);
  not not_15 (not_15_out, PHI0_out);
  not not_16 (not_16_out, PHI0_out);
  nor nor_14 (nor_14_out, nor_10_out, nor_13_out);
  D_LATCH d_latch_15 (.EN(PHI0_out), .in(nor_11_out), .out(d_latch_15_out));  // open: out_2
  D_LATCH d_latch_16 (.EN(not_15_out), .in(nor_12_out), .out(d_latch_16_out));  // open: out_2
  D_LATCH d_latch_17 (.EN(not_16_out), .in(nor_14_out), .out_2(d_latch_17_out_2));  // open: out
  not not_17 (not_17_out, nor_14_out);
  not not_18 (not_18_out, d_latch_18_out);
  D_LATCH d_latch_18 (.EN(PHI0_out), .in(d_latch_17_out_2), .out(d_latch_18_out));  // open: out_2
  nand nand_3 (nand_3_out, d_latch_19_out, nready);
  or or_1 (or_1_out, not_18_out, nready);
  nand nand_4 (nand_4_out, d_latch_21_out, nready);
  or or_2 (or_2_out, not_23_out, nready);
  nand nand_5 (nand_5_out, d_latch_23_out, nready);
  or or_3 (or_3_out, not_24_out, nready);
  nand nand_6 (nand_6_out, d_latch_25_out, nready);
  or or_4 (or_4_out, not_25_out, nready);
  nor nor_15 (nor_15_out, d_latch_13_out_2, d_latch_20_out);
  and and_5 (and_5_out, nand_3_out, or_1_out);
  nor nor_16 (nor_16_out, d_latch_13_out_2, d_latch_22_out);
  and and_6 (and_6_out, nand_4_out, or_2_out);
  nor nor_17 (nor_17_out, d_latch_13_out_2, d_latch_24_out);
  and and_7 (and_7_out, nand_5_out, or_3_out);
  nor nor_18 (nor_18_out, d_latch_13_out_2, d_latch_26_out);
  and and_8 (and_8_out, nand_6_out, or_4_out);
  D_LATCH d_latch_19 (.EN(PHI0_out), .in(nor_15_out), .out(d_latch_19_out));  // open: out_2
  not not_19 (not_19_out, PHI0_out);
  D_LATCH d_latch_20 (.EN(not_19_out), .in(and_5_out), .out(d_latch_20_out));  // open: out_2
  D_LATCH d_latch_21 (.EN(PHI0_out), .in(nor_16_out), .out(d_latch_21_out));  // open: out_2
  D_LATCH d_latch_22 (.EN(not_20_out), .in(and_6_out), .out(d_latch_22_out));  // open: out_2
  not not_20 (not_20_out, PHI0_out);
  D_LATCH d_latch_23 (.EN(PHI0_out), .in(nor_17_out), .out(d_latch_23_out));  // open: out_2
  not not_21 (not_21_out, PHI0_out);
  D_LATCH d_latch_24 (.EN(not_21_out), .in(and_7_out), .out(d_latch_24_out));  // open: out_2
  D_LATCH d_latch_25 (.EN(PHI0_out), .in(nor_18_out), .out(d_latch_25_out));  // open: out_2
  D_LATCH d_latch_26 (.EN(not_22_out), .in(and_8_out), .out(d_latch_26_out));  // open: out_2
  not not_22 (not_22_out, PHI0_out);
  not not_23 (not_23_out, d_latch_19_out);
  not not_24 (not_24_out, d_latch_21_out);
  not not_25 (not_25_out, d_latch_23_out);
  not not_26 (nT2, nor_15_out);
  not not_27 (nT3, nor_16_out);
  not not_28 (nT4, nor_17_out);
  not not_29 (nT5, nor_18_out);

  // Notes on the sheet:
  //   /ready
  //   TRESX
  //   T0
  //   /ready
  //   TRES1
  //   T1
  //   /BRTAKEN
  //   BR2
  //   91/92
  //   /ready
  //   ENDX
  //   /ready
  //   ENDS
  //   BRFW
  //   ACR
  //   /ready
  //   RESP
  //   TRESX
  //   ENDS
  //   /T0X
  //   T0
  //   /T1X
  //   TRES2
  //   /ready
  //   ENDS
  //   /ready
  //   RESP
  //   T1
  //   T1
  //   TRES1
  //   TRES2
  //   /ready
  //   TRES2
  //   TRES2
  //   TRES2
  //   /T2
  //   /T3
  //   /T4
  //   /T5
endmodule

module FLAGS (
  input  PHI0,
  input  DB0,
  input  DB1,
  input  DB2,
  input  DB3,
  input  DB4,
  input  DB5,
  input  DB6,
  input  DB7,
  input  P_DB,
  input  DB_P,
  input  DBZ_Z,
  input  DB_N,
  input  IR5_C,
  input  ACR_C,
  input  DB_C,
  input  IR5_D,
  input  IR5_I,
  input  AVR_V,
  input  DB_V,
  input  _0_V,
  input  _1_V,
  input  nIR5,
  input  ACR,
  input  AVR,
  input  B_OUT,
  output DB0_2,
  output DB1_2,
  output DB2_2,
  output DB3_2,
  output DB4_2,
  output DB5_2,
  output DB6_2,
  output DB7_2,
  output nZ_OUT,
  output nN_OUT,
  output nC_OUT,
  output nD_OUT,
  output nI_OUT,
  output nV_OUT
);

  wire and_1_out, and_2_out, and_3_out, and_4_out, and_5_out, d_latch_1_out_2, d_latch_2_out_2,
       d_latch_3_out, d_latch_4_out, d_latch_5_out, d_latch_6_out, multiplexer_1_out, multiplexer_2_out,
       nand_1_out, nand_2_out, nand_3_out, nand_4_out, nand_5_out, nand_6_out, nand_7_out, nand_8_out,
       nand_9_out, nand_10_out, nand_11_out, nand_12_out, nand_13_out, nand_14_out, nand_15_out, nand_16_out,
       nor_1_out, nor_2_out, nor_3_out, nor_4_out, nor_5_out, not_1_out, not_2_out, not_3_out, not_4_out,
       not_5_out, not_6_out, not_7_out, not_8_out, not_9_out, not_10_out, not_11_out, not_12_out, not_13_out,
       not_14_out, not_15_out, not_16_out, not_17_out, not_18_out, not_19_out, not_20_out, not_21_out,
       not_22_out, or_1_out;

  nor nor_1 (nor_1_out, DB0, DB1, DB2, DB3, DB4, DB5, DB6, DB7);
  not not_1 (not_1_out, nor_1_out);
  not not_2 (not_2_out, ACR);
  not not_3 (not_3_out, DB0);
  nor nor_2 (nor_2_out, IR5_C, ACR_C, DB_C);
  not not_4 (not_4_out, DB3);
  nor nor_3 (nor_3_out, IR5_D, DB_P);
  not not_5 (not_5_out, DB2);
  nor nor_4 (nor_4_out, IR5_I, DB_P);
  not not_6 (not_6_out, AVR);
  not not_7 (not_7_out, DB6);
  nor nor_5 (nor_5_out, AVR_V, _1_V, DB_V);
  not not_8 (not_8_out, DB1);
  not not_9 (not_9_out, DB7);
  nand nand_1 (nand_1_out, nIR5, IR5_C);
  nand nand_2 (nand_2_out, not_2_out, ACR_C);
  nand nand_3 (nand_3_out, not_3_out, DB_C);
  nand nand_4 (nand_4_out, d_latch_3_out, nor_2_out);
  nand nand_5 (nand_5_out, nIR5, IR5_D);
  nand nand_6 (nand_6_out, not_4_out, DB_P);
  nand nand_7 (nand_7_out, d_latch_4_out, nor_3_out);
  nand nand_8 (nand_8_out, nIR5, IR5_I);
  nand nand_9 (nand_9_out, not_5_out, DB_P);
  nand nand_10 (nand_10_out, d_latch_5_out, nor_4_out);
  nand nand_11 (nand_11_out, not_6_out, AVR_V);
  nand nand_12 (nand_12_out, not_7_out, DB_V);
  nand nand_13 (nand_13_out, d_latch_6_out, nor_5_out);
  not not_10 (not_10_out, _0_V);
  or or_1 (or_1_out, DBZ_Z, DB_P);
  nand nand_14 (nand_14_out, not_1_out, DBZ_Z);
  and and_1 (and_1_out, nand_14_out, nand_15_out);
  nand nand_15 (nand_15_out, not_8_out, DB_P);
  nand nand_16 (nand_16_out, not_9_out, DB_N);
  and and_2 (and_2_out, nand_1_out, nand_2_out, nand_3_out, nand_4_out);
  and and_3 (and_3_out, nand_5_out, nand_6_out, nand_7_out);
  and and_4 (and_4_out, nand_8_out, nand_9_out, nand_10_out);
  and and_5 (and_5_out, nand_11_out, nand_12_out, nand_13_out, not_10_out);
  Multiplexer multiplexer_1 (
    .in0(d_latch_1_out_2), .in1(and_1_out), .out(multiplexer_1_out), .sel(or_1_out));  // open: en
  D_LATCH d_latch_1 (.EN(PHI0), .in(nZ_OUT), .out_2(d_latch_1_out_2));  // open: out
  Multiplexer multiplexer_2 (
    .in0(d_latch_2_out_2), .in1(nand_16_out), .out(multiplexer_2_out), .sel(DB_N));  // open: en
  D_LATCH d_latch_2 (.EN(PHI0), .in(nN_OUT), .out_2(d_latch_2_out_2));  // open: out
  D_LATCH d_latch_3 (.EN(PHI0), .in(nC_OUT), .out(d_latch_3_out));  // open: out_2
  D_LATCH d_latch_4 (.EN(PHI0), .in(nD_OUT), .out(d_latch_4_out));  // open: out_2
  D_LATCH d_latch_5 (.EN(PHI0), .in(nI_OUT), .out(d_latch_5_out));  // open: out_2
  D_LATCH d_latch_6 (.EN(PHI0), .in(nV_OUT), .out(d_latch_6_out));  // open: out_2
  not not_11 (not_11_out, PHI0);
  D_LATCH d_latch_7 (.EN(not_11_out), .in(multiplexer_1_out), .out_2(nZ_OUT));  // open: out
  D_LATCH d_latch_8 (.EN(not_12_out), .in(multiplexer_2_out), .out_2(nN_OUT));  // open: out
  not not_12 (not_12_out, PHI0);
  D_LATCH d_latch_9 (.EN(not_13_out), .in(and_2_out), .out_2(nC_OUT));  // open: out
  not not_13 (not_13_out, PHI0);
  not not_14 (not_14_out, PHI0);
  D_LATCH d_latch_10 (.EN(not_14_out), .in(and_3_out), .out_2(nD_OUT));  // open: out
  D_LATCH d_latch_11 (.EN(not_15_out), .in(and_4_out), .out_2(nI_OUT));  // open: out
  not not_15 (not_15_out, PHI0);
  D_LATCH d_latch_12 (.EN(not_16_out), .in(and_5_out), .out_2(nV_OUT));  // open: out
  not not_16 (not_16_out, PHI0);
  assign DB0_2 = P_DB ? not_17_out : 1'bz;  // Controlled_Buffer controlled_buffer_1
  not not_17 (not_17_out, nC_OUT);
  not not_18 (not_18_out, nZ_OUT);
  assign DB1_2 = P_DB ? not_18_out : 1'bz;  // Controlled_Buffer controlled_buffer_2
  not not_19 (not_19_out, nI_OUT);
  assign DB2_2 = P_DB ? not_19_out : 1'bz;  // Controlled_Buffer controlled_buffer_3
  not not_20 (not_20_out, nD_OUT);
  assign DB3_2 = P_DB ? not_20_out : 1'bz;  // Controlled_Buffer controlled_buffer_4
  assign DB4_2 = P_DB ? B_OUT : 1'bz;  // Controlled_Buffer controlled_buffer_5
  assign DB6_2 = P_DB ? not_21_out : 1'bz;  // Controlled_Buffer controlled_buffer_6
  not not_21 (not_21_out, nV_OUT);
  assign DB7_2 = P_DB ? not_22_out : 1'bz;  // Controlled_Buffer controlled_buffer_7
  not not_22 (not_22_out, nN_OUT);

  // Notes on the sheet:
  //   ACR/C
  //   1/V
  //   /DBZ
  //   IR5/C
  //   DB/C
  //   IR5/D
  //   DB/P
  //   IR5/I
  //   DB/P
  //   AVR/V
  //   DB/V
  //   /IR5
  //   IR5/C
  //   /ACR
  //   ACR/C
  //   /DB0
  //   DB/C
  //   /IR5
  //   IR5/D
  //   /DB3
  //   DB/P
  //   /IR5
  //   IR5/I
  //   /DB2
  //   DB/P
  //   /AVR
  //   AVR/V
  //   /DB6
  //   DB/V
  //   0/V
  //   DBZ/Z
  //   DB/P
  //   /DBZ
  //   DBZ/Z
  //   /DB1
  //   DB/P
  //   /DB7
  //   DB/N
  //   DB/N
  //   Z FLAG
  //   N FLAG
  //   C FLAG
  //   D FLAG
  //   I FLAG
  //   V FLAG
  //   /Z_OUT
  //   /N_OUT
  //   /C_OUT
  //   /D_OUT
  //   /I_OUT
  //   /V_OUT
  //   N.C.
endmodule

module BUSES (
  input  PHI0,
  input  DATA0,
  input  DATA1,
  input  DATA2,
  input  DATA3,
  input  DATA4,
  input  DATA5,
  input  DATA6,
  input  DATA7,
  input  SB0,
  input  SB1,
  input  SB2,
  input  SB3,
  input  SB4,
  input  SB5,
  input  SB6,
  input  SB7,
  input  DB0,
  input  DB1,
  input  DB2,
  input  DB3,
  input  DB4,
  input  DB5,
  input  DB6,
  input  DB7,
  input  ADL0,
  input  ADL1,
  input  ADL2,
  input  ADL3,
  input  ADL4,
  input  ADL5,
  input  ADL6,
  input  ADL7,
  input  ADH0,
  input  ADH1,
  input  ADH2,
  input  ADH3,
  input  ADH4,
  input  ADH5,
  input  ADH6,
  input  ADH7,
  input  _0_ADL0,
  input  _0_ADL1,
  input  _0_ADL2,
  input  ADL_ABL,
  input  ADH_ABH,
  input  SB_DB,
  input  SB_ADH,
  input  _0_ADH0,
  input  _0_ADH17,
  input  DL_ADL,
  input  DL_ADH,
  input  DL_DB,
  input  RD,
  output DATA0_2,
  output DATA1_2,
  output DATA2_2,
  output DATA3_2,
  output DATA4_2,
  output DATA5_2,
  output DATA6_2,
  output DATA7_2,
  output SB0_2,
  output SB1_2,
  output SB2_2,
  output SB3_2,
  output SB4_2,
  output SB5_2,
  output SB6_2,
  output SB7_2,
  output DB0_2,
  output DB1_2,
  output DB2_2,
  output DB3_2,
  output DB4_2,
  output DB5_2,
  output DB6_2,
  output DB7_2,
  output ADL0_2,
  output ADL1_2,
  output ADL2_2,
  output ADL3_2,
  output ADL4_2,
  output ADL5_2,
  output ADL6_2,
  output ADL7_2,
  output ADH0_2,
  output ADH1_2,
  output ADH2_2,
  output ADH3_2,
  output ADH4_2,
  output ADH5_2,
  output ADH6_2,
  output ADH7_2,
  output ADDR0,
  output ADDR1,
  output ADDR2,
  output ADDR3,
  output ADDR4,
  output ADDR5,
  output ADDR6,
  output ADDR7,
  output ADDR8,
  output ADDR9,
  output ADDR10,
  output ADDR11,
  output ADDR12,
  output ADDR13,
  output ADDR14,
  output ADDR15
);

  wire and_1_out, and_2_out, and_3_out, and_4_out, and_5_out, and_6_out, and_7_out, and_8_out, and_9_out,
       and_10_out, and_11_out, controlled_buffer_3_out, d_latch_1_out_2, d_latch_2_out_2, not_1_out,
       not_2_out, not_3_out, not_4_out, not_5_out, not_6_out, not_7_out, not_8_out, not_9_out, not_10_out,
       not_11_out, not_12_out, not_13_out, not_14_out, not_15_out, not_16_out, not_17_out, not_18_out,
       not_19_out, not_20_out, not_21_out, not_22_out;

  not not_1 (not_1_out, DATA0);
  not not_2 (not_2_out, PHI0);
  D_LATCH d_latch_1 (.EN(PHI0), .in(not_1_out), .out_2(d_latch_1_out_2));  // open: out
  D_LATCH d_latch_2 (.EN(not_3_out), .in(not_4_out), .out_2(d_latch_2_out_2));  // open: out
  not not_3 (not_3_out, PHI0);
  not not_4 (not_4_out, DB0);
  assign ADH0_2 = SB_DB ? SB0 : 1'bz;  // Controlled_Buffer controlled_buffer_1
  assign ADH0_2 = SB_ADH ? SB0 : 1'bz;  // Controlled_Buffer controlled_buffer_2
  assign controlled_buffer_3_out = not_2_out ? d_latch_1_out_2 : 1'bz;  // Controlled_Buffer controlled_buffer_3
  not not_5 (not_5_out, RD);
  assign ADH0_2 = DL_ADL ? controlled_buffer_3_out : 1'bz;  // Controlled_Buffer controlled_buffer_4
  assign ADH0_2 = DL_ADH ? controlled_buffer_3_out : 1'bz;  // Controlled_Buffer controlled_buffer_5
  assign ADH0_2 = DL_DB ? controlled_buffer_3_out : 1'bz;  // Controlled_Buffer controlled_buffer_6
  assign DATA0_2 = not_5_out ? d_latch_2_out_2 : 1'bz;  // Controlled_Buffer controlled_buffer_7
  BUSKEEPER buskeeper_1 (.io(ADH0_2));
  BUSKEEPER buskeeper_2 (.io(ADH0_2));
  BUSKEEPER buskeeper_3 (.io(ADH0_2));
  BUSKEEPER buskeeper_4 (.io(ADH0_2));
  not not_6 (not_6_out, _0_ADL0);
  not not_7 (not_7_out, _0_ADL1);
  not not_8 (not_8_out, _0_ADL2);
  not not_9 (not_9_out, _0_ADH0);
  not not_10 (not_10_out, _0_ADH17);
  not not_11 (not_11_out, PHI0);
  and and_1 (and_1_out, ADL0, not_6_out);
  not not_12 (not_12_out, and_1_out);
  not not_13 (not_13_out, PHI0);
  not not_14 (not_14_out, and_2_out);
  and and_2 (and_2_out, ADL1, not_7_out);
  not not_15 (not_15_out, PHI0);
  not not_16 (not_16_out, and_3_out);
  and and_3 (and_3_out, ADL2, not_8_out);
  not not_17 (not_17_out, PHI0);
  not not_18 (not_18_out, ADL3);
  not not_19 (not_19_out, PHI0);
  and and_4 (and_4_out, ADH0, not_9_out);
  not not_20 (not_20_out, and_4_out);
  not not_21 (not_21_out, PHI0);
  not not_22 (not_22_out, and_5_out);
  and and_5 (and_5_out, ADH1, not_10_out);
  and and_6 (and_6_out, not_11_out, ADL_ABL);
  and and_7 (and_7_out, not_13_out, ADL_ABL);
  and and_8 (and_8_out, not_15_out, ADL_ABL);
  and and_9 (and_9_out, not_17_out, ADL_ABL);
  and and_10 (and_10_out, not_19_out, ADH_ABH);
  and and_11 (and_11_out, not_21_out, ADH_ABH);
  D_Flip_Flop #(.trigger("high")) d_ff_1 (.clk(and_6_out), .D(not_12_out), .Q(ADDR0));  // open: Qn, preset, en, reset
  D_Flip_Flop #(.trigger("high")) d_ff_2 (.clk(and_7_out), .D(not_14_out), .Q(ADDR1));  // open: Qn, preset, en, reset
  D_Flip_Flop #(.trigger("high")) d_ff_3 (.clk(and_8_out), .D(not_16_out), .Q(ADDR2));  // open: Qn, preset, en, reset
  D_Flip_Flop #(.trigger("high")) d_ff_4 (.clk(and_9_out), .D(not_18_out), .Q(ADDR3));  // open: Qn, preset, en, reset
  D_Flip_Flop #(.trigger("high")) d_ff_5 (.clk(and_10_out), .D(not_20_out), .Q(ADDR8));  // open: Qn, preset, en, reset
  D_Flip_Flop #(.trigger("high")) d_ff_6 (.clk(and_11_out), .D(not_22_out), .Q(ADDR9));  // open: Qn, preset, en, reset
  assign ADH0_2 = PHI0 ? 1'b1 : 1'bz;  // Controlled_Buffer controlled_buffer_8

  assign ADL0_2 = ADH0_2;
  assign DB0_2 = ADH0_2;
  assign SB0_2 = ADH0_2;

  // Notes on the sheet:
  //   DATA0...7
  //   DB0...7
  //   SB/DB
  //   SB/ADH
  //   RD
  //   DL/ADL
  //   DL/ADH
  //   DL/DB
  //   0/ADL0
  //   0/ADL2
  //   0/ADL2
  //   0/ADH0
  //   0/ADH17
  //   DATA LATCH
  //   DATA0...7
  //   ADL0
  //   ADL1
  //   ADL2
  //   ADL3...7
  //   ADH0
  //   ADH1...7
  //   ADL/ABL
  //   ADL/ABL
  //   ADL/ABL
  //   ADL/ABL
  //   ADH/ABH
  //   ADH/ABH
  //   PRECHARGE
endmodule

module BUSKEEPER (
  input  io
);

  wire not_2_out;

  not not_1 (io, not_2_out);
  not not_2 (not_2_out, io);
endmodule
module PC (
  input  _1_PC,
  input  PCL_PCL,
  input  PCL_ADL,
  input  ADL_PCL,
  input  PCL_DB,
  input  PCH_PCH,
  input  PCH_ADH,
  input  ADH_PCH,
  input  PCH_DB
);

  wire and_1_out, and_2_out, and_3_out, and_4_out, and_5_out, and_6_out, and_7_out, and_8_out,
       controlled_buffer_1_out, controlled_buffer_3_out, controlled_buffer_5_out, controlled_buffer_7_out,
       controlled_buffer_9_out, controlled_buffer_11_out, controlled_buffer_13_out, controlled_buffer_15_out,
       controlled_buffer_17_out, controlled_buffer_18_out, controlled_buffer_19_out,
       controlled_buffer_20_out, controlled_buffer_21_out, controlled_buffer_22_out,
       controlled_buffer_23_out, controlled_buffer_24_out, controlled_buffer_25_out,
       controlled_buffer_26_out, controlled_buffer_27_out, controlled_buffer_28_out,
       controlled_buffer_29_out, controlled_buffer_30_out, controlled_buffer_31_out,
       controlled_buffer_32_out, controlled_buffer_33_out, controlled_buffer_35_out,
       controlled_buffer_37_out, controlled_buffer_39_out, controlled_buffer_41_out,
       controlled_buffer_43_out, controlled_buffer_45_out, controlled_buffer_47_out,
       controlled_buffer_49_out, controlled_buffer_50_out, controlled_buffer_51_out,
       controlled_buffer_52_out, controlled_buffer_53_out, controlled_buffer_54_out,
       controlled_buffer_55_out, controlled_buffer_56_out, controlled_buffer_57_out,
       controlled_buffer_58_out, controlled_buffer_59_out, controlled_buffer_60_out,
       controlled_buffer_61_out, controlled_buffer_62_out, controlled_buffer_63_out,
       controlled_buffer_64_out, d_ff_1_q, d_ff_2_qn, d_ff_3_q, d_ff_4_qn, d_ff_5_q, d_ff_6_qn, d_ff_7_q,
       d_ff_8_qn, d_ff_9_q, d_ff_10_q, d_ff_11_q, d_ff_12_q, d_ff_13_q, d_ff_14_q, d_ff_15_q, d_ff_16_q,
       d_ff_17_qn, d_ff_18_q, d_ff_19_qn, d_ff_20_q, d_ff_21_qn, d_ff_22_q, d_ff_23_qn, d_ff_24_q, d_ff_25_q,
       d_ff_26_q, d_ff_27_q, d_ff_28_q, d_ff_29_q, d_ff_30_q, d_ff_31_q, d_ff_32_q, nand_1_out, nand_2_out,
       nand_3_out, nand_4_out, nand_5_out, nand_6_out, nand_7_out, nand_8_out, nand_9_out, nand_10_out,
       nand_11_out, nand_12_out, nand_13_out, nand_14_out, nand_15_out, nand_16_out, nor_1_out, nor_2_out,
       nor_3_out, nor_4_out, nor_5_out, nor_6_out, nor_7_out, nor_8_out, nor_9_out, nor_10_out, nor_11_out,
       nor_12_out, nor_13_out, nor_14_out, nor_15_out, nor_16_out, nor_17_out, nor_18_out, not_1_out,
       not_2_out, not_3_out, not_4_out, not_5_out, not_6_out, not_7_out, not_8_out, not_9_out, not_10_out,
       not_11_out, not_12_out, not_13_out, not_14_out, not_15_out, not_16_out, not_17_out, not_18_out,
       not_19_out, not_20_out, not_21_out, not_22_out, not_23_out, not_24_out, not_25_out, not_26_out,
       not_27_out, not_28_out, not_29_out, not_30_out, not_31_out, not_32_out, not_33_out, not_34_out,
       not_35_out, not_36_out, not_37_out, not_38_out, not_39_out, not_40_out, not_41_out, not_42_out,
       not_43_out, not_44_out, not_45_out, not_46_out, not_47_out, not_48_out, not_49_out, or_1_out,
       or_2_out, or_3_out, or_4_out, or_5_out, or_6_out, or_7_out, or_8_out, PHI0_out, undriven, undriven_2,
       undriven_3, undriven_4, undriven_5, undriven_6, undriven_7, undriven_8, undriven_9, undriven_10,
       undriven_11, undriven_12, undriven_13, undriven_14, undriven_15, undriven_16;

  Clock PHI0 (.out(PHI0_out));
  not not_1 (not_1_out, not_18_out);
  not not_2 (not_2_out, not_20_out);
  not not_3 (not_3_out, not_22_out);
  not not_4 (not_4_out, not_24_out);
  nand nand_1 (nand_1_out, _1_PC, not_17_out);
  and and_1 (and_1_out, nand_1_out, not_5_out);
  not not_5 (not_5_out, nor_5_out);
  nor nor_1 (nor_1_out, nor_5_out, not_1_out);
  or or_1 (or_1_out, nor_1_out, not_6_out);
  not not_6 (not_6_out, nand_5_out);
  nand nand_2 (nand_2_out, nand_5_out, not_19_out);
  and and_2 (and_2_out, nand_2_out, not_7_out);
  not not_7 (not_7_out, nor_6_out);
  nor nor_2 (nor_2_out, nor_6_out, not_2_out);
  or or_2 (or_2_out, nor_2_out, not_8_out);
  not not_8 (not_8_out, nand_6_out);
  nand nand_3 (nand_3_out, nand_6_out, not_21_out);
  and and_3 (and_3_out, nand_3_out, not_9_out);
  not not_9 (not_9_out, nor_7_out);
  nor nor_3 (nor_3_out, nor_7_out, not_3_out);
  or or_3 (or_3_out, nor_3_out, not_10_out);
  not not_10 (not_10_out, nand_7_out);
  nand nand_4 (nand_4_out, nand_7_out, not_23_out);
  and and_4 (and_4_out, nand_4_out, not_11_out);
  not not_11 (not_11_out, nor_8_out);
  nor nor_4 (nor_4_out, nor_8_out, not_4_out);
  or or_4 (or_4_out, nor_4_out, not_12_out);
  not not_12 (not_12_out, nand_8_out);
  D_Flip_Flop #(.trigger("falling")) d_ff_1 (
    .clk(PHI0_out), .D(and_1_out), .Q(d_ff_1_q));  // open: Qn, preset, en, reset
  nor nor_5 (nor_5_out, _1_PC, not_17_out);
  D_Flip_Flop #(.trigger("falling")) d_ff_2 (
    .clk(PHI0_out), .D(or_1_out), .Qn(d_ff_2_qn));  // open: Q, preset, en, reset
  nand nand_5 (nand_5_out, nor_5_out, not_13_out);
  not not_13 (not_13_out, not_18_out);
  D_Flip_Flop #(.trigger("falling")) d_ff_3 (
    .clk(PHI0_out), .D(and_2_out), .Q(d_ff_3_q));  // open: Qn, preset, en, reset
  nor nor_6 (nor_6_out, nand_5_out, not_19_out);
  D_Flip_Flop #(.trigger("falling")) d_ff_4 (
    .clk(PHI0_out), .D(or_2_out), .Qn(d_ff_4_qn));  // open: Q, preset, en, reset
  nand nand_6 (nand_6_out, nor_6_out, not_14_out);
  not not_14 (not_14_out, not_20_out);
  D_Flip_Flop #(.trigger("falling")) d_ff_5 (
    .clk(PHI0_out), .D(and_3_out), .Q(d_ff_5_q));  // open: Qn, preset, en, reset
  nor nor_7 (nor_7_out, nand_6_out, not_21_out);
  D_Flip_Flop #(.trigger("falling")) d_ff_6 (
    .clk(PHI0_out), .D(or_3_out), .Qn(d_ff_6_qn));  // open: Q, preset, en, reset
  nand nand_7 (nand_7_out, nor_7_out, not_15_out);
  not not_15 (not_15_out, not_22_out);
  D_Flip_Flop #(.trigger("falling")) d_ff_7 (
    .clk(PHI0_out), .D(and_4_out), .Q(d_ff_7_q));  // open: Qn, preset, en, reset
  nor nor_8 (nor_8_out, nand_7_out, not_23_out);
  D_Flip_Flop #(.trigger("falling")) d_ff_8 (
    .clk(PHI0_out), .D(or_4_out), .Qn(d_ff_8_qn));  // open: Q, preset, en, reset
  nand nand_8 (nand_8_out, nor_8_out, not_16_out);
  not not_16 (not_16_out, not_24_out);
  assign controlled_buffer_1_out = PCL_PCL ? d_ff_1_q : 1'bz;  // Controlled_Buffer controlled_buffer_1
  assign controlled_buffer_1_out = ADL_PCL ? undriven : 1'bz;  // Controlled_Buffer controlled_buffer_2
  not not_17 (not_17_out, d_ff_9_q);
  assign controlled_buffer_3_out = PCL_PCL ? d_ff_2_qn : 1'bz;  // Controlled_Buffer controlled_buffer_3
  assign controlled_buffer_3_out = ADL_PCL ? undriven_2 : 1'bz;  // Controlled_Buffer controlled_buffer_4
  not not_18 (not_18_out, d_ff_10_q);
  assign controlled_buffer_5_out = PCL_PCL ? d_ff_3_q : 1'bz;  // Controlled_Buffer controlled_buffer_5
  assign controlled_buffer_5_out = ADL_PCL ? undriven_3 : 1'bz;  // Controlled_Buffer controlled_buffer_6
  not not_19 (not_19_out, d_ff_11_q);
  assign controlled_buffer_7_out = PCL_PCL ? d_ff_4_qn : 1'bz;  // Controlled_Buffer controlled_buffer_7
  assign controlled_buffer_7_out = ADL_PCL ? undriven_4 : 1'bz;  // Controlled_Buffer controlled_buffer_8
  not not_20 (not_20_out, d_ff_12_q);
  assign controlled_buffer_9_out = PCL_PCL ? d_ff_5_q : 1'bz;  // Controlled_Buffer controlled_buffer_9
  assign controlled_buffer_9_out = ADL_PCL ? undriven_5 : 1'bz;  // Controlled_Buffer controlled_buffer_10
  not not_21 (not_21_out, d_ff_13_q);
  assign controlled_buffer_11_out = PCL_PCL ? d_ff_6_qn : 1'bz;  // Controlled_Buffer controlled_buffer_11
  assign controlled_buffer_11_out = ADL_PCL ? undriven_6 : 1'bz;  // Controlled_Buffer controlled_buffer_12
  not not_22 (not_22_out, d_ff_14_q);
  assign controlled_buffer_13_out = PCL_PCL ? d_ff_7_q : 1'bz;  // Controlled_Buffer controlled_buffer_13
  assign controlled_buffer_13_out = ADL_PCL ? undriven_7 : 1'bz;  // Controlled_Buffer controlled_buffer_14
  not not_23 (not_23_out, d_ff_15_q);
  assign controlled_buffer_15_out = PCL_PCL ? d_ff_8_qn : 1'bz;  // Controlled_Buffer controlled_buffer_15
  assign controlled_buffer_15_out = ADL_PCL ? undriven_8 : 1'bz;  // Controlled_Buffer controlled_buffer_16
  not not_24 (not_24_out, d_ff_16_q);
  Controlled_Buffer controlled_buffer_17 (.in(d_ff_1_q), .out(controlled_buffer_17_out));  // open: en
  Controlled_Buffer controlled_buffer_18 (.in(d_ff_1_q), .out(controlled_buffer_18_out));  // open: en
  D_Flip_Flop #(.trigger("high")) d_ff_9 (
    .clk(1'b1), .D(controlled_buffer_1_out), .Q(d_ff_9_q));  // open: Qn, preset, en, reset
  Controlled_Buffer controlled_buffer_19 (.in(d_ff_2_qn), .out(controlled_buffer_19_out));  // open: en
  Controlled_Buffer controlled_buffer_20 (.in(d_ff_2_qn), .out(controlled_buffer_20_out));  // open: en
  D_Flip_Flop #(.trigger("high")) d_ff_10 (
    .clk(1'b1), .D(controlled_buffer_3_out), .Q(d_ff_10_q));  // open: Qn, preset, en, reset
  Controlled_Buffer controlled_buffer_21 (.in(d_ff_3_q), .out(controlled_buffer_21_out));  // open: en
  Controlled_Buffer controlled_buffer_22 (.in(d_ff_3_q), .out(controlled_buffer_22_out));  // open: en
  D_Flip_Flop #(.trigger("high")) d_ff_11 (
    .clk(1'b1), .D(controlled_buffer_5_out), .Q(d_ff_11_q));  // open: Qn, preset, en, reset
  Controlled_Buffer controlled_buffer_23 (.in(d_ff_4_qn), .out(controlled_buffer_23_out));  // open: en
  Controlled_Buffer controlled_buffer_24 (.in(d_ff_4_qn), .out(controlled_buffer_24_out));  // open: en
  D_Flip_Flop #(.trigger("high")) d_ff_12 (
    .clk(1'b1), .D(controlled_buffer_7_out), .Q(d_ff_12_q));  // open: Qn, preset, en, reset
  Controlled_Buffer controlled_buffer_25 (.in(d_ff_5_q), .out(controlled_buffer_25_out));  // open: en
  Controlled_Buffer controlled_buffer_26 (.in(d_ff_5_q), .out(controlled_buffer_26_out));  // open: en
  D_Flip_Flop #(.trigger("high")) d_ff_13 (
    .clk(1'b1), .D(controlled_buffer_9_out), .Q(d_ff_13_q));  // open: Qn, preset, en, reset
  Controlled_Buffer controlled_buffer_27 (.in(d_ff_6_qn), .out(controlled_buffer_27_out));  // open: en
  Controlled_Buffer controlled_buffer_28 (.in(d_ff_6_qn), .out(controlled_buffer_28_out));  // open: en
  D_Flip_Flop #(.trigger("high")) d_ff_14 (
    .clk(1'b1), .D(controlled_buffer_11_out), .Q(d_ff_14_q));  // open: Qn, preset, en, reset
  Controlled_Buffer controlled_buffer_29 (.in(d_ff_7_q), .out(controlled_buffer_29_out));  // open: en
  Controlled_Buffer controlled_buffer_30 (.in(d_ff_7_q), .out(controlled_buffer_30_out));  // open: en
  D_Flip_Flop #(.trigger("high")) d_ff_15 (
    .clk(1'b1), .D(controlled_buffer_13_out), .Q(d_ff_15_q));  // open: Qn, preset, en, reset
  Controlled_Buffer controlled_buffer_31 (.in(d_ff_8_qn), .out(controlled_buffer_31_out));  // open: en
  Controlled_Buffer controlled_buffer_32 (.in(d_ff_8_qn), .out(controlled_buffer_32_out));  // open: en
  D_Flip_Flop #(.trigger("high")) d_ff_16 (
    .clk(1'b1), .D(controlled_buffer_15_out), .Q(d_ff_16_q));  // open: Qn, preset, en, reset
  nor nor_9 (nor_9_out, not_17_out, not_18_out, not_19_out, not_20_out, not_21_out, not_22_out, not_23_out, not_24_out);
  not not_25 (not_25_out, not_41_out);
  not not_26 (not_26_out, not_43_out);
  not not_27 (not_27_out, not_45_out);
  not not_28 (not_28_out, not_47_out);
  nor nor_10 (nor_10_out, nor_9_out, not_25_out);
  not not_29 (not_29_out, nand_13_out);
  nand nand_9 (nand_9_out, nand_13_out, not_42_out);
  not not_30 (not_30_out, nor_14_out);
  nor nor_11 (nor_11_out, nor_14_out, not_26_out);
  not not_31 (not_31_out, nand_14_out);
  nand nand_10 (nand_10_out, nand_14_out, not_44_out);
  not not_32 (not_32_out, nor_15_out);
  nor nor_12 (nor_12_out, nor_18_out, not_27_out);
  not not_33 (not_33_out, nand_15_out);
  nand nand_11 (nand_11_out, nand_15_out, not_46_out);
  not not_34 (not_34_out, nor_16_out);
  nor nor_13 (nor_13_out, nor_16_out, not_28_out);
  not not_35 (not_35_out, nand_16_out);
  nand nand_12 (nand_12_out, nand_16_out, not_48_out);
  not not_36 (not_36_out, nor_17_out);
  or or_5 (or_5_out, nor_10_out, not_29_out);
  nand nand_13 (nand_13_out, nor_9_out, not_37_out);
  and and_5 (and_5_out, nand_9_out, not_30_out);
  nor nor_14 (nor_14_out, nand_13_out, not_42_out);
  or or_6 (or_6_out, nor_11_out, not_31_out);
  nand nand_14 (nand_14_out, nor_14_out, not_38_out);
  and and_6 (and_6_out, nand_10_out, not_32_out);
  nor nor_15 (nor_15_out, nand_14_out, not_44_out);
  or or_7 (or_7_out, nor_12_out, not_33_out);
  nand nand_15 (nand_15_out, nor_18_out, not_39_out);
  and and_7 (and_7_out, nand_11_out, not_34_out);
  nor nor_16 (nor_16_out, nand_15_out, not_46_out);
  or or_8 (or_8_out, nor_13_out, not_35_out);
  nand nand_16 (nand_16_out, nor_16_out, not_40_out);
  and and_8 (and_8_out, nand_12_out, not_36_out);
  nor nor_17 (nor_17_out, nand_16_out, not_48_out);
  D_Flip_Flop #(.trigger("falling")) d_ff_17 (
    .clk(PHI0_out), .D(or_5_out), .Qn(d_ff_17_qn));  // open: Q, preset, en, reset
  not not_37 (not_37_out, not_41_out);
  D_Flip_Flop #(.trigger("falling")) d_ff_18 (
    .clk(PHI0_out), .D(and_5_out), .Q(d_ff_18_q));  // open: Qn, preset, en, reset
  D_Flip_Flop #(.trigger("falling")) d_ff_19 (
    .clk(PHI0_out), .D(or_6_out), .Qn(d_ff_19_qn));  // open: Q, preset, en, reset
  not not_38 (not_38_out, not_43_out);
  D_Flip_Flop #(.trigger("falling")) d_ff_20 (
    .clk(PHI0_out), .D(and_6_out), .Q(d_ff_20_q));  // open: Qn, preset, en, reset
  D_Flip_Flop #(.trigger("falling")) d_ff_21 (
    .clk(PHI0_out), .D(or_7_out), .Qn(d_ff_21_qn));  // open: Q, preset, en, reset
  not not_39 (not_39_out, not_45_out);
  D_Flip_Flop #(.trigger("falling")) d_ff_22 (
    .clk(PHI0_out), .D(and_7_out), .Q(d_ff_22_q));  // open: Qn, preset, en, reset
  D_Flip_Flop #(.trigger("falling")) d_ff_23 (
    .clk(PHI0_out), .D(or_8_out), .Qn(d_ff_23_qn));  // open: Q, preset, en, reset
  not not_40 (not_40_out, not_47_out);
  D_Flip_Flop #(.trigger("falling")) d_ff_24 (
    .clk(PHI0_out), .D(and_8_out), .Q(d_ff_24_q));  // open: Qn, preset, en, reset
  assign controlled_buffer_33_out = PCH_PCH ? d_ff_17_qn : 1'bz;  // Controlled_Buffer controlled_buffer_33
  assign controlled_buffer_33_out = ADH_PCH ? undriven_9 : 1'bz;  // Controlled_Buffer controlled_buffer_34
  not not_41 (not_41_out, d_ff_25_q);
  assign controlled_buffer_35_out = PCH_PCH ? d_ff_18_q : 1'bz;  // Controlled_Buffer controlled_buffer_35
  assign controlled_buffer_35_out = ADH_PCH ? undriven_10 : 1'bz;  // Controlled_Buffer controlled_buffer_36
  not not_42 (not_42_out, d_ff_26_q);
  assign controlled_buffer_37_out = PCH_PCH ? d_ff_19_qn : 1'bz;  // Controlled_Buffer controlled_buffer_37
  assign controlled_buffer_37_out = ADH_PCH ? undriven_11 : 1'bz;  // Controlled_Buffer controlled_buffer_38
  not not_43 (not_43_out, d_ff_27_q);
  assign controlled_buffer_39_out = PCH_PCH ? d_ff_20_q : 1'bz;  // Controlled_Buffer controlled_buffer_39
  assign controlled_buffer_39_out = ADH_PCH ? undriven_12 : 1'bz;  // Controlled_Buffer controlled_buffer_40
  not not_44 (not_44_out, d_ff_28_q);
  assign controlled_buffer_41_out = PCH_PCH ? d_ff_21_qn : 1'bz;  // Controlled_Buffer controlled_buffer_41
  assign controlled_buffer_41_out = ADH_PCH ? undriven_13 : 1'bz;  // Controlled_Buffer controlled_buffer_42
  not not_45 (not_45_out, d_ff_29_q);
  assign controlled_buffer_43_out = PCH_PCH ? d_ff_22_q : 1'bz;  // Controlled_Buffer controlled_buffer_43
  assign controlled_buffer_43_out = ADH_PCH ? undriven_14 : 1'bz;  // Controlled_Buffer controlled_buffer_44
  not not_46 (not_46_out, d_ff_30_q);
  assign controlled_buffer_45_out = PCH_PCH ? d_ff_23_qn : 1'bz;  // Controlled_Buffer controlled_buffer_45
  assign controlled_buffer_45_out = ADH_PCH ? undriven_15 : 1'bz;  // Controlled_Buffer controlled_buffer_46
  not not_47 (not_47_out, d_ff_31_q);
  assign controlled_buffer_47_out = PCH_PCH ? d_ff_24_q : 1'bz;  // Controlled_Buffer controlled_buffer_47
  assign controlled_buffer_47_out = ADH_PCH ? undriven_16 : 1'bz;  // Controlled_Buffer controlled_buffer_48
  not not_48 (not_48_out, d_ff_32_q);
  Controlled_Buffer controlled_buffer_49 (.in(d_ff_17_qn), .out(controlled_buffer_49_out));  // open: en
  Controlled_Buffer controlled_buffer_50 (.in(d_ff_17_qn), .out(controlled_buffer_50_out));  // open: en
  D_Flip_Flop #(.trigger("high")) d_ff_25 (
    .clk(1'b1), .D(controlled_buffer_33_out), .Q(d_ff_25_q));  // open: Qn, preset, en, reset
  Controlled_Buffer controlled_buffer_51 (.in(d_ff_18_q), .out(controlled_buffer_51_out));  // open: en
  Controlled_Buffer controlled_buffer_52 (.in(d_ff_18_q), .out(controlled_buffer_52_out));  // open: en
  D_Flip_Flop #(.trigger("high")) d_ff_26 (
    .clk(1'b1), .D(controlled_buffer_35_out), .Q(d_ff_26_q));  // open: Qn, preset, en, reset
  Controlled_Buffer controlled_buffer_53 (.in(d_ff_19_qn), .out(controlled_buffer_53_out));  // open: en
  Controlled_Buffer controlled_buffer_54 (.in(d_ff_19_qn), .out(controlled_buffer_54_out));  // open: en
  D_Flip_Flop #(.trigger("high")) d_ff_27 (
    .clk(1'b1), .D(controlled_buffer_37_out), .Q(d_ff_27_q));  // open: Qn, preset, en, reset
  Controlled_Buffer controlled_buffer_55 (.in(d_ff_20_q), .out(controlled_buffer_55_out));  // open: en
  Controlled_Buffer controlled_buffer_56 (.in(d_ff_20_q), .out(controlled_buffer_56_out));  // open: en
  D_Flip_Flop #(.trigger("falling")) d_ff_28 (
    .clk(1'b1), .D(controlled_buffer_39_out), .Q(d_ff_28_q));  // open: Qn, preset, en, reset
  Controlled_Buffer controlled_buffer_57 (.in(d_ff_21_qn), .out(controlled_buffer_57_out));  // open: en
  Controlled_Buffer controlled_buffer_58 (.in(d_ff_21_qn), .out(controlled_buffer_58_out));  // open: en
  D_Flip_Flop #(.trigger("falling")) d_ff_29 (
    .clk(1'b1), .D(controlled_buffer_41_out), .Q(d_ff_29_q));  // open: Qn, preset, en, reset
  Controlled_Buffer controlled_buffer_59 (.in(d_ff_22_q), .out(controlled_buffer_59_out));  // open: en
  Controlled_Buffer controlled_buffer_60 (.in(d_ff_22_q), .out(controlled_buffer_60_out));  // open: en
  D_Flip_Flop #(.trigger("falling")) d_ff_30 (
    .clk(1'b1), .D(controlled_buffer_43_out), .Q(d_ff_30_q));  // open: Qn, preset, en, reset
  Controlled_Buffer controlled_buffer_61 (.in(d_ff_23_qn), .out(controlled_buffer_61_out));  // open: en
  Controlled_Buffer controlled_buffer_62 (.in(d_ff_23_qn), .out(controlled_buffer_62_out));  // open: en
  D_Flip_Flop #(.trigger("falling")) d_ff_31 (
    .clk(1'b1), .D(controlled_buffer_45_out), .Q(d_ff_31_q));  // open: Qn, preset, en, reset
  Controlled_Buffer controlled_buffer_63 (.in(d_ff_24_q), .out(controlled_buffer_63_out));  // open: en
  Controlled_Buffer controlled_buffer_64 (.in(d_ff_24_q), .out(controlled_buffer_64_out));  // open: en
  D_Flip_Flop #(.trigger("falling")) d_ff_32 (
    .clk(1'b1), .D(controlled_buffer_47_out), .Q(d_ff_32_q));  // open: Qn, preset, en, reset
  not not_49 (not_49_out, nor_9_out);
  nor nor_18 (nor_18_out, not_49_out, not_41_out, not_42_out, not_43_out, not_44_out);

  // Notes on the sheet:
  //   carry
  //   carry
  //   carry
  //   carry
  //   carry
  //   carry
  //   carry
  //   carry
  //   carry
  //   carry
  //   carry
  //   carry
  //   carry
  //   carry
  //   carry
  //   carry
  //   PCL/PCL
  //   ADL/PCL
  //   PCL/PCL
  //   ADL/PCL
  //   PCL/PCL
  //   ADL/PCL
  //   PCL/PCL
  //   ADL/PCL
  //   PCL/PCL
  //   ADL/PCL
  //   PCL/PCL
  //   ADL/PCL
  //   PCL/PCL
  //   ADL/PCL
  //   PCL/PCL
  //   ADL/PCL
  //   PCL
  //   PCL/DB
  //   PCL/ADL
  //   PCL/DB
  //   PCL/ADL
  //   PCL/DB
  //   PCL/ADL
  //   PCL/DB
  //   PCL/ADL
  //   PCL/DB
  //   PCL/ADL
  //   PCL/DB
  //   PCL/ADL
  //   PCL/DB
  //   PCL/ADL
  //   PCL/DB
  //   PCL/ADL
  //   PCLC
  //   carry
  //   carry
  //   carry
  //   carry
  //   carry
  //   carry
  //   carry
  //   carry
  //   carry
  //   carry
  //   carry
  //   carry
  //   carry
  //   carry
  //   carry
  //   carry
  //   PCH/PCH
  //   ADH/PCH
  //   PCH/PCH
  //   ADH/PCH
  //   PCH/PCH
  //   ADH/PCH
  //   PCH/PCH
  //   ADH/PCH
  //   PCH/PCH
  //   ADH/PCH
  //   PCH/PCH
  //   ADH/PCH
  //   PCH/PCH
  //   ADH/PCH
  //   PCH/PCH
  //   ADH/PCH
  //   PCH0-3
  //   PCH4-7
  //   PCH/DB
  //   PCH/ADH
  //   PCH/DB
  //   PCH/ADH
  //   PCH/DB
  //   PCH/ADH
  //   PCH/DB
  //   PCH/ADH
  //   PCH/DB
  //   PCH/ADH
  //   PCH/DB
  //   PCH/ADH
  //   PCH/DB
  //   PCH/ADH
  //   PCH/DB
  //   PCH/ADH
  //   PCHC
endmodule
