// Logisim project LFO.circ as structural Verilog: 3 circuits, main circuit main
module main (
  input  PHI,
  input  RES,
  input  D6,
  input  D7,
  input  nR4015,
  input  W4017,
  input  Z1,
  output ACLK,
  output nACLK,
  output LFOINT,
  output D6_2,
  output _240HZ,
  output _120HZ
);

  wire and_1_out, and_2_out, and_3_out, and_4_out, CLK_out, counter_1_q, d_ff_1_qn, d_ff_2_q, dlatch_1_nout,
       dlatch_2_nout, dlatch_3_nout, dlatch_3_out, dlatch_4_nout, dlatch_5_nout, dlatch_6_nout,
       dlatch_7_nout, dlatch_8_nout, dlatch_9_nout, dlatch_10_nout, dlatch_11_nout, dlatch_12_nout,
       dlatch_13_nout, dlatch_14_nout, dlatch_15_nout, dlatch_16_nout, dlatch_17_nout, dlatch_18_nout,
       dlatch_19_nout, dlatch_19_out, dlatch_20_nout, dlatch_20_out, dlatch_21_nout, dlatch_21_out,
       dlatch_22_nout, dlatch_22_out, dlatch_23_nout, dlatch_23_out, dlatch_24_nout, dlatch_24_out,
       dlatch_25_nout, dlatch_25_out, dlatch_26_nout, dlatch_26_out, dlatch_27_nout, dlatch_27_out,
       dlatch_28_nout, dlatch_28_out, dlatch_29_nout, dlatch_29_out, dlatch_30_nout, dlatch_30_out,
       dlatch_31_nout, dlatch_31_out, dlatch_32_nout, dlatch_32_out, dlatch_33_nout, dlatch_33_out,
       multiplexer_3_out, nand_1_out, nor_1_out, nor_2_out, nor_3_out, nor_4_out, nor_5_out, nor_6_out,
       nor_7_out, nor_8_out, nor_9_out, nor_10_out, not_1_out, not_2_out, not_3_out, not_4_out, not_5_out,
       or_1_out, or_2_out;

  Clock #(.highDuration(4), .lowDuration(4)) CLK (.out(CLK_out));
  not not_1 (not_1_out, CLK_out);
  or or_1 (or_1_out, W4017, RES);
  DLATCH dlatch_1 (.EN(CLK_out), .in(1'b0), .nout(dlatch_1_nout));  // open: out
  Counter #(.width(1), .max('h1)) counter_1 (
    .Q(counter_1_q), .clk(nACLK), .clr(or_1_out));  // open: load, D, count, carry
  DLATCH dlatch_2 (.EN(not_1_out), .in(dlatch_1_nout), .nout(dlatch_2_nout));  // open: out
  and and_1 (and_1_out, ACLK, W4017);
  D_Flip_Flop #(.trigger("high")) d_ff_1 (.clk(and_1_out), .D(D7), .Qn(d_ff_1_qn));  // open: Q, preset, en, reset
  and and_2 (and_2_out, ACLK, W4017);
  D_Flip_Flop #(.trigger("high")) d_ff_2 (.clk(and_2_out), .D(D6), .Q(d_ff_2_q));  // open: Qn, preset, en, reset
  not not_2 (not_2_out, dlatch_2_nout);
  DLATCH dlatch_3 (.EN(nACLK), .in(d_ff_1_qn), .out(dlatch_3_out), .nout(dlatch_3_nout));
  Multiplexer multiplexer_1 (.in0(1'b0), .in1(not_2_out), .out(nACLK), .sel(CLK_out));  // open: en
  not not_3 (not_3_out, CLK_out);
  Multiplexer multiplexer_2 (.in0(not_3_out), .in1(1'b0), .out(ACLK), .sel(1'b0));  // open: en
  nor nor_1 (nor_1_out, dlatch_3_out, Z1);
  DLATCH dlatch_4 (.EN(multiplexer_3_out), .in(and_4_out), .nout(dlatch_4_nout));  // open: out
  DLATCH dlatch_5 (.EN(multiplexer_3_out), .in(dlatch_19_nout), .nout(dlatch_5_nout));  // open: out
  DLATCH dlatch_6 (.EN(multiplexer_3_out), .in(dlatch_20_nout), .nout(dlatch_6_nout));  // open: out
  DLATCH dlatch_7 (.EN(multiplexer_3_out), .in(dlatch_21_nout), .nout(dlatch_7_nout));  // open: out
  DLATCH dlatch_8 (.EN(multiplexer_3_out), .in(dlatch_22_nout), .nout(dlatch_8_nout));  // open: out
  DLATCH dlatch_9 (.EN(multiplexer_3_out), .in(dlatch_23_nout), .nout(dlatch_9_nout));  // open: out
  DLATCH dlatch_10 (.EN(multiplexer_3_out), .in(dlatch_24_nout), .nout(dlatch_10_nout));  // open: out
  DLATCH dlatch_11 (.EN(multiplexer_3_out), .in(dlatch_25_nout), .nout(dlatch_11_nout));  // open: out
  DLATCH dlatch_12 (.EN(multiplexer_3_out), .in(dlatch_26_nout), .nout(dlatch_12_nout));  // open: out
  DLATCH dlatch_13 (.EN(multiplexer_3_out), .in(dlatch_27_nout), .nout(dlatch_13_nout));  // open: out
  DLATCH dlatch_14 (.EN(multiplexer_3_out), .in(dlatch_28_nout), .nout(dlatch_14_nout));  // open: out
  DLATCH dlatch_15 (.EN(multiplexer_3_out), .in(dlatch_29_nout), .nout(dlatch_15_nout));  // open: out
  DLATCH dlatch_16 (.EN(multiplexer_3_out), .in(dlatch_30_nout), .nout(dlatch_16_nout));  // open: out
  DLATCH dlatch_17 (.EN(multiplexer_3_out), .in(dlatch_31_nout), .nout(dlatch_17_nout));  // open: out
  DLATCH dlatch_18 (.EN(multiplexer_3_out), .in(dlatch_32_nout), .nout(dlatch_18_nout));  // open: out
  DLATCH dlatch_19 (.EN(nACLK), .in(dlatch_4_nout), .out(dlatch_19_out), .nout(dlatch_19_nout));
  DLATCH dlatch_20 (.EN(nACLK), .in(dlatch_5_nout), .out(dlatch_20_out), .nout(dlatch_20_nout));
  DLATCH dlatch_21 (.EN(nACLK), .in(dlatch_6_nout), .out(dlatch_21_out), .nout(dlatch_21_nout));
  DLATCH dlatch_22 (.EN(nACLK), .in(dlatch_7_nout), .out(dlatch_22_out), .nout(dlatch_22_nout));
  DLATCH dlatch_23 (.EN(nACLK), .in(dlatch_8_nout), .out(dlatch_23_out), .nout(dlatch_23_nout));
  DLATCH dlatch_24 (.EN(nACLK), .in(dlatch_9_nout), .out(dlatch_24_out), .nout(dlatch_24_nout));
  DLATCH dlatch_25 (.EN(nACLK), .in(dlatch_10_nout), .out(dlatch_25_out), .nout(dlatch_25_nout));
  DLATCH dlatch_26 (.EN(nACLK), .in(dlatch_11_nout), .out(dlatch_26_out), .nout(dlatch_26_nout));
  DLATCH dlatch_27 (.EN(nACLK), .in(dlatch_12_nout), .out(dlatch_27_out), .nout(dlatch_27_nout));
  DLATCH dlatch_28 (.EN(nACLK), .in(dlatch_13_nout), .out(dlatch_28_out), .nout(dlatch_28_nout));
  DLATCH dlatch_29 (.EN(nACLK), .in(dlatch_14_nout), .out(dlatch_29_out), .nout(dlatch_29_nout));
  DLATCH dlatch_30 (.EN(nACLK), .in(dlatch_15_nout), .out(dlatch_30_out), .nout(dlatch_30_nout));
  DLATCH dlatch_31 (.EN(nACLK), .in(dlatch_16_nout), .out(dlatch_31_out), .nout(dlatch_31_nout));
  DLATCH dlatch_32 (.EN(nACLK), .in(dlatch_17_nout), .out(dlatch_32_out), .nout(dlatch_32_nout));
  DLATCH dlatch_33 (.EN(nACLK), .in(dlatch_18_nout), .out(dlatch_33_out), .nout(dlatch_33_nout));
  or or_2 (or_2_out, nor_5_out, nor_6_out, Z1);
  Multiplexer multiplexer_3 (.in0(or_2_out), .in1(1'b0), .out(multiplexer_3_out), .sel(nACLK));  // open: en
  nor nor_2 (nor_2_out, dlatch_19_out, dlatch_20_nout, dlatch_21_nout, dlatch_22_nout, dlatch_23_nout, dlatch_24_out, dlatch_25_out, dlatch_26_nout, dlatch_27_nout, dlatch_28_nout, dlatch_29_nout, dlatch_30_nout, dlatch_31_out, dlatch_32_nout, dlatch_33_nout);
  nor nor_3 (nor_3_out, dlatch_19_out, dlatch_20_out, dlatch_21_nout, dlatch_22_nout, dlatch_23_nout, dlatch_24_nout, dlatch_25_nout, dlatch_26_nout, dlatch_27_nout, dlatch_28_out, dlatch_29_out, dlatch_30_nout, dlatch_31_out, dlatch_32_out, dlatch_33_nout);
  nor nor_4 (nor_4_out, dlatch_19_out, dlatch_20_out, dlatch_21_nout, dlatch_22_nout, dlatch_23_out, dlatch_24_nout, dlatch_25_out, dlatch_26_out, dlatch_27_nout, dlatch_28_nout, dlatch_29_out, dlatch_30_out, dlatch_31_nout, dlatch_32_out, dlatch_33_nout);
  nor nor_5 (nor_5_out, dlatch_19_out, dlatch_20_out, dlatch_21_out, dlatch_22_out, dlatch_23_out, dlatch_24_nout, dlatch_25_nout, dlatch_26_nout, dlatch_27_nout, dlatch_28_out, dlatch_29_nout, dlatch_30_out, dlatch_31_nout, dlatch_32_nout, dlatch_32_nout, dlatch_3_nout);
  nor nor_6 (nor_6_out, dlatch_19_out, dlatch_20_nout, dlatch_21_out, dlatch_22_nout, dlatch_23_nout, dlatch_24_nout, dlatch_25_nout, dlatch_26_out, dlatch_27_out, dlatch_28_nout, dlatch_29_nout, dlatch_30_nout, dlatch_31_out, dlatch_32_out, dlatch_33_out);
  nor nor_7 (nor_7_out, dlatch_19_nout, dlatch_20_nout, dlatch_21_nout, dlatch_22_nout, dlatch_23_nout, dlatch_24_nout, dlatch_25_nout, dlatch_26_nout, dlatch_27_nout, dlatch_28_nout, dlatch_29_nout, dlatch_30_nout, dlatch_31_nout, dlatch_32_nout, dlatch_33_nout);
  nand nand_1 (nand_1_out, dlatch_32_nout, dlatch_33_nout);
  nor nor_8 (nor_8_out, nor_7_out, dlatch_33_nout);
  not not_4 (not_4_out, dlatch_32_nout);
  not not_5 (not_5_out, and_3_out);
  and and_3 (and_3_out, nor_8_out, not_4_out);
  and and_4 (and_4_out, nand_1_out, not_5_out);
  nor nor_9 (nor_9_out, nor_1_out, nor_2_out, nor_3_out, nor_4_out, nor_5_out, nor_6_out);
  nor nor_10 (nor_10_out, nor_1_out, nor_3_out, nor_5_out, nor_6_out);
  or or_3 (_240HZ, ACLK, nor_9_out);
  or or_4 (_120HZ, ACLK, nor_10_out);

  // Notes on the sheet:
  //   PHI1
  //   PHI2
  //   ACLK
  //   TIMING (REDUNDAND)
  //   CONTROL
  //   Z2
  //   0
  //   1
  //   2
  //   3
  //   4
  //   5
  //   6
  //   7
  //   8
  //   9
  //   10
  //   11
  //   12
  //   13
  //   14
  //   C14
  //   C13
  //   DIVIDER
  //   APU CLOCK
endmodule

module DLATCH (
  input  EN,
  input  in,
  output out,
  output nout
);

  D_Flip_Flop #(.trigger("high")) d_ff_1 (.clk(EN), .D(in), .Q(out), .Qn(nout));  // open: preset, en, reset
endmodule

module LFO_counter (
  input  STEP_RELOAD,
  input  CARRY_IN,
  input  RES,
  input  W4017
);

  wire ACLK_out, dlatch_1_nout, dlatch_1_out, multiplexer_1_out, not_1_out, not_2_out;

  Clock ACLK (.out(ACLK_out));
  Multiplexer multiplexer_1 (.in0(1'b1), .in1(CARRY_IN), .out(multiplexer_1_out), .sel(STEP_RELOAD));  // open: en
  not not_1 (not_1_out, ACLK_out);
  DLATCH dlatch_1 (.EN(ACLK_out), .in(not_2_out), .out(dlatch_1_out), .nout(dlatch_1_nout));
  not not_2 (not_2_out, multiplexer_1_out);
endmodule
