// Logisim project 6502_Evo.circ as structural Verilog: 43 circuits, main circuit MOS_6502
module MOS_6502 (
  input  n_NMI,
  input  n_IRQ,
  input  RDY,
  input  n_RES,
  input  SO,
  input  D0_IN,
  input  D1_IN,
  input  D2_IN,
  input  D3_IN,
  input  D4_IN,
  input  D5_IN,
  input  D6_IN,
  input  D7_IN,
  output PHI1,
  output PHI2,
  output R_W,
  output SYNC,
  output A0,
  output A1,
  output A2,
  output A3,
  output A4,
  output A5,
  output A6,
  output A7,
  output D0_OUT,
  output D1_OUT,
  output D2_OUT,
  output D3_OUT,
  output D4_OUT,
  output D5_OUT,
  output A8,
  output A9,
  output A10,
  output A11,
  output A12,
  output A13,
  output A14,
  output A15,
  output D6_OUT,
  output D7_OUT
);

  wire alu_1_acr, alu_1_avr, d_ff_1_qn, d_ff_2_qn, d_ff_3_q, d_latch_1_not_q, d_latch_2_not_q,
       d_latch_3_not_q, d_latch_4_not_q, decoder_trans_1_l_0_090b2452, decoder_trans_1_l_1_28cbbb7d,
       decoder_trans_1_l_2_143403ae, decoder_trans_1_l_3_39a566ac, decoder_trans_1_l_4_558283f2,
       decoder_trans_1_l_5_9518e519, decoder_trans_1_l_6_5b7e39b9, decoder_trans_1_l_7_14ab2533,
       decoder_trans_1_l_8_05eb4f56, decoder_trans_1_l_9_0082242d, decoder_trans_1_l_10_57b0d741,
       decoder_trans_1_l_11_aa2e7fa3, decoder_trans_1_l_12_85a3418f, decoder_trans_1_l_13_587da886,
       decoder_trans_1_l_14_4f483598, decoder_trans_1_l_15_5dad5732, decoder_trans_1_l_16_c7396848,
       decoder_trans_1_l_17_0f5278c7, decoder_trans_1_l_18_4ab117a9, decoder_trans_1_l_19_e094c090,
       decoder_trans_1_l_20_adeacd1b, decoder_trans_1_l_21_ada5c31c, decoder_trans_1_l_22_f545d19e,
       decoder_trans_1_l_23_d0835dd9, decoder_trans_1_l_24_b6efc2f4, decoder_trans_1_l_25_f5ad6aee,
       decoder_trans_1_l_26_ffeee2da, decoder_trans_1_l_27_6492a6f4, decoder_trans_1_l_28_647e552a,
       decoder_trans_1_l_29_1d3a3eb3, decoder_trans_1_l_30_3bf8f3d0, decoder_trans_1_l_31_e958c8e2,
       decoder_trans_1_l_32_7de83e69, decoder_trans_1_l_33_cae225fb, decoder_trans_1_l_34_97db28cb,
       decoder_trans_1_l_35_8b2262aa, decoder_trans_1_l_36_34609549, decoder_trans_1_l_37_acfb42d2,
       decoder_trans_1_l_38_43aa51c3, decoder_trans_1_l_39_c97a3f22, decoder_trans_1_l_40_1e6b68e0,
       decoder_trans_1_l_41_b24af141, decoder_trans_1_l_42_ae8bf3e0, decoder_trans_1_l_43_fdaf143b,
       decoder_trans_1_l_44_bb416d4b, decoder_trans_1_l_45_e516ed8c, decoder_trans_1_l_46_6c10990a,
       decoder_trans_1_l_47_7c60183d, decoder_trans_1_l_48_330a6f3f, decoder_trans_1_l_49_f70f8148,
       decoder_trans_1_l_50_6b408103, decoder_trans_1_l_51_79fb832a, decoder_trans_1_l_52_253f2da2,
       decoder_trans_1_l_53_d08b6e35, decoder_trans_1_l_54_01afe50f, decoder_trans_1_l_55_73ecc214,
       decoder_trans_1_l_56_35bf93dd, decoder_trans_1_l_57_0f0af090, decoder_trans_1_l_58_4e7562c2,
       decoder_trans_1_l_59_d4e3d539, decoder_trans_1_l_60_8c46ae22, decoder_trans_1_l_61_ef440803,
       decoder_trans_1_l_62_1470bf03, decoder_trans_1_l_63_0a5e7e38, decoder_trans_1_l_64_e6cb4ce5,
       decoder_trans_1_l_65_6a42b4dc, decoder_trans_1_l_66_3306dbdf, decoder_trans_1_l_67_7ef59d0e,
       decoder_trans_1_l_68_820561b0, decoder_trans_1_l_69_cbdecb8a, decoder_trans_1_l_70_099188dc,
       decoder_trans_1_l_71_facae7ec, decoder_trans_1_l_72_92460769, decoder_trans_1_l_73_3c19a6e4,
       decoder_trans_1_l_74_b252c222, decoder_trans_1_l_75_7b13a6b0, decoder_trans_1_l_76_ea80c3c2,
       decoder_trans_1_l_77_f96dcb28, decoder_trans_1_l_78_8a0d457e, decoder_trans_1_l_79_7d8df45e,
       decoder_trans_1_l_80_053c0a7a, decoder_trans_1_l_81_2726249e, decoder_trans_1_l_82_298ac22b,
       decoder_trans_1_l_83_79a418b7, decoder_trans_1_l_84_e79a1766, decoder_trans_1_l_85_b2daf010,
       decoder_trans_1_l_86_b98cc819, decoder_trans_1_l_87_c637b311, decoder_trans_1_l_88_055bb603,
       decoder_trans_1_l_89_5d5fe4c7, decoder_trans_1_l_90_55afaa76, decoder_trans_1_l_91_d03b9369,
       decoder_trans_1_l_92_0cc1d36a, decoder_trans_1_l_93_eaf60893, decoder_trans_1_l_94_95326b03,
       decoder_trans_1_l_95_f060a0fd, decoder_trans_1_l_96_3d015798, decoder_trans_1_l_97_f3e813cd,
       decoder_trans_1_l_98_f4cee2ae, decoder_trans_1_l_99_bb939962, decoder_trans_1_l_100_16b00339,
       decoder_trans_1_l_101_c09bb9ac, decoder_trans_1_l_102_614a85bf, decoder_trans_1_l_103_52940b9a,
       decoder_trans_1_l_104_443c5ff0, decoder_trans_1_l_105_5ce959fd, decoder_trans_1_l_106_2a9581c6,
       decoder_trans_1_l_107_a96ffaba, decoder_trans_1_l_108_c205b5ff, decoder_trans_1_l_109_2fe88a94,
       decoder_trans_1_l_110_4cc555bd, decoder_trans_1_l_111_2b81c3c9, decoder_trans_1_l_112_708a0f10,
       decoder_trans_1_l_113_fbaa75ad, decoder_trans_1_l_114_f9625e87, decoder_trans_1_l_115_b1986fe2,
       decoder_trans_1_l_116_0ba24dc4, decoder_trans_1_l_117_10a3c8b1, decoder_trans_1_l_118_e0e8abfe,
       decoder_trans_1_l_119_86db347d, decoder_trans_1_l_120_c53a083f, decoder_trans_1_l_121_da158f44,
       decoder_trans_1_l_122_0e8f1988, decoder_trans_1_l_123_a8638cda, decoder_trans_1_l_124_8d81fffd,
       decoder_trans_1_l_125_8f968e43, decoder_trans_1_l_126_7e3003c6, decoder_trans_1_l_127_28942974,
       decoder_trans_1_l_128_23d7200b, decoder_trans_1_l_129_7b5e5edf, ir_1_ir0, ir_1_ir1, ir_1_ir2,
       ir_1_ir3, ir_1_ir4, ir_1_ir5, ir_1_ir6, ir_1_ir7, not_1_out, not_2_out, not_3_out, PHI0_out,
       predecode_1_l_implied_b029c4af, predecode_1_l_pd0_ff4f5362, predecode_1_l_pd1_2bbb5f50,
       predecode_1_l_pd2_b780aebe, predecode_1_l_pd3_595d30b7, predecode_1_l_pd4_d7b0250f,
       predecode_1_l_pd5_1b763385, predecode_1_l_pd6_cacfa412, predecode_1_l_pd7_1b7e0f3f,
       predecode_1_l_twocycle_54b4f369, random_logic_1_acr_c_5cb02b46, random_logic_1_db_c_01ed158e,
       random_logic_1_db_n_68ba26fc, random_logic_1_db_p_37e5c1ba, random_logic_1_db_v_92adf01b,
       random_logic_1_dbz_z_a7859eb1, random_logic_1_ends, random_logic_1_endx, random_logic_1_fetch,
       random_logic_1_ir5_c_8cbf3e52, random_logic_1_ir5_d_ec89b364, random_logic_1_ir5_i_e7eeeda5,
       random_logic_1_l_0_ir_c32b8001, random_logic_1_l_0_v_f0a8dd83, random_logic_1_l_c_out_f91ece9c,
       random_logic_1_l_d_out_7d61c6e7, random_logic_1_l_i_out_6792f219, random_logic_1_l_n_out_10df9d15,
       random_logic_1_l_t0_5a901129, random_logic_1_l_t1x_624de7e6, random_logic_1_l_t2_37fe4d42,
       random_logic_1_l_t3_3fe619b3, random_logic_1_l_t4_d9b6e407, random_logic_1_l_t5_89b31bc6,
       random_logic_1_l_v_out_959779aa, random_logic_1_l_z_out_2813b2ba, random_logic_1_p_db_42279b60,
       random_logic_1_r_w_47630a0a, random_logic_1_rd, random_logic_1_t1, random_logic_1_tres1,
       random_logic_1_tresx, random_logic_1_wr;
  wire [2:0] random_logic_1_dl_adl_6c5e0116, random_logic_1_l_acin_e173f520;
  wire [4:0] random_logic_1_adl_abl_5bea59e2;
  wire [6:0] random_logic_1_sb_ac_b159eec5;
  wire [7:0] alu_1_ac_debug, alu_1_add_debug, alu_1_adh0, alu_1_ai_debug, alu_1_bi_debug, dl_1_dl_debug,
       dl_1_dor_debug, random_logic_1_db0, random_logic_1_y_sb_d628d28f, regs_1_adl0, regs_1_s_debug,
       regs_1_sb0_out, regs_1_x_debug, regs_1_y_debug;
  wire [8:0] random_logic_1_adh_pch_61520abf;
  wire [12:0] random_logic_1_ndb_add_ee0a1870;
  wire [15:0] pc_1_pc_debug, pc_1_pcs_debug;

  buf buffer_1 (SYNC, random_logic_1_t1);
  D_Flip_Flop #(.trigger("high")) d_ff_1 (.D(n_NMI), .clk(PHI2), .Qn(d_ff_1_qn));  // open: Q, preset, reset
  DECODER_TRANS decoder_trans_1 (
    .L_10_57b0d741(decoder_trans_1_l_10_57b0d741), .L_11_aa2e7fa3(decoder_trans_1_l_11_aa2e7fa3),
    .L_12_85a3418f(decoder_trans_1_l_12_85a3418f), .L_13_587da886(decoder_trans_1_l_13_587da886),
    .L_14_4f483598(decoder_trans_1_l_14_4f483598), .L_15_5dad5732(decoder_trans_1_l_15_5dad5732),
    .L_16_c7396848(decoder_trans_1_l_16_c7396848), .L_17_0f5278c7(decoder_trans_1_l_17_0f5278c7),
    .L_18_4ab117a9(decoder_trans_1_l_18_4ab117a9), .L_19_e094c090(decoder_trans_1_l_19_e094c090),
    .L_20_adeacd1b(decoder_trans_1_l_20_adeacd1b), .L_21_ada5c31c(decoder_trans_1_l_21_ada5c31c),
    .L_22_f545d19e(decoder_trans_1_l_22_f545d19e), .L_23_d0835dd9(decoder_trans_1_l_23_d0835dd9),
    .L_24_b6efc2f4(decoder_trans_1_l_24_b6efc2f4), .L_25_f5ad6aee(decoder_trans_1_l_25_f5ad6aee),
    .L_26_ffeee2da(decoder_trans_1_l_26_ffeee2da), .L_27_6492a6f4(decoder_trans_1_l_27_6492a6f4),
    .L_28_647e552a(decoder_trans_1_l_28_647e552a), .L_29_1d3a3eb3(decoder_trans_1_l_29_1d3a3eb3),
    .L_30_3bf8f3d0(decoder_trans_1_l_30_3bf8f3d0), .L_31_e958c8e2(decoder_trans_1_l_31_e958c8e2),
    .L_32_7de83e69(decoder_trans_1_l_32_7de83e69), .L_33_cae225fb(decoder_trans_1_l_33_cae225fb),
    .L_34_97db28cb(decoder_trans_1_l_34_97db28cb), .L_35_8b2262aa(decoder_trans_1_l_35_8b2262aa),
    .L_36_34609549(decoder_trans_1_l_36_34609549), .L_37_acfb42d2(decoder_trans_1_l_37_acfb42d2),
    .L_38_43aa51c3(decoder_trans_1_l_38_43aa51c3), .L_39_c97a3f22(decoder_trans_1_l_39_c97a3f22),
    .L_40_1e6b68e0(decoder_trans_1_l_40_1e6b68e0), .L_41_b24af141(decoder_trans_1_l_41_b24af141),
    .L_42_ae8bf3e0(decoder_trans_1_l_42_ae8bf3e0), .L_43_fdaf143b(decoder_trans_1_l_43_fdaf143b),
    .L_44_bb416d4b(decoder_trans_1_l_44_bb416d4b), .L_0_090b2452(decoder_trans_1_l_0_090b2452),
    .L_45_e516ed8c(decoder_trans_1_l_45_e516ed8c), .L_46_6c10990a(decoder_trans_1_l_46_6c10990a),
    .L_47_7c60183d(decoder_trans_1_l_47_7c60183d), .L_48_330a6f3f(decoder_trans_1_l_48_330a6f3f),
    .L_49_f70f8148(decoder_trans_1_l_49_f70f8148), .L_50_6b408103(decoder_trans_1_l_50_6b408103),
    .L_51_79fb832a(decoder_trans_1_l_51_79fb832a), .L_52_253f2da2(decoder_trans_1_l_52_253f2da2),
    .L_53_d08b6e35(decoder_trans_1_l_53_d08b6e35), .L_1_28cbbb7d(decoder_trans_1_l_1_28cbbb7d),
    .L_54_01afe50f(decoder_trans_1_l_54_01afe50f), .L_55_73ecc214(decoder_trans_1_l_55_73ecc214),
    .L_56_35bf93dd(decoder_trans_1_l_56_35bf93dd), .L_57_0f0af090(decoder_trans_1_l_57_0f0af090),
    .L_58_4e7562c2(decoder_trans_1_l_58_4e7562c2), .L_59_d4e3d539(decoder_trans_1_l_59_d4e3d539),
    .L_60_8c46ae22(decoder_trans_1_l_60_8c46ae22), .L_61_ef440803(decoder_trans_1_l_61_ef440803),
    .L_62_1470bf03(decoder_trans_1_l_62_1470bf03), .L_2_143403ae(decoder_trans_1_l_2_143403ae),
    .L_63_0a5e7e38(decoder_trans_1_l_63_0a5e7e38), .L_64_e6cb4ce5(decoder_trans_1_l_64_e6cb4ce5),
    .L_65_6a42b4dc(decoder_trans_1_l_65_6a42b4dc), .L_66_3306dbdf(decoder_trans_1_l_66_3306dbdf),
    .L_67_7ef59d0e(decoder_trans_1_l_67_7ef59d0e), .L_68_820561b0(decoder_trans_1_l_68_820561b0),
    .L_69_cbdecb8a(decoder_trans_1_l_69_cbdecb8a), .L_70_099188dc(decoder_trans_1_l_70_099188dc),
    .L_71_facae7ec(decoder_trans_1_l_71_facae7ec), .L_72_92460769(decoder_trans_1_l_72_92460769),
    .L_3_39a566ac(decoder_trans_1_l_3_39a566ac), .L_73_3c19a6e4(decoder_trans_1_l_73_3c19a6e4),
    .L_74_b252c222(decoder_trans_1_l_74_b252c222), .L_75_7b13a6b0(decoder_trans_1_l_75_7b13a6b0),
    .L_76_ea80c3c2(decoder_trans_1_l_76_ea80c3c2), .L_77_f96dcb28(decoder_trans_1_l_77_f96dcb28),
    .L_78_8a0d457e(decoder_trans_1_l_78_8a0d457e), .L_79_7d8df45e(decoder_trans_1_l_79_7d8df45e),
    .L_80_053c0a7a(decoder_trans_1_l_80_053c0a7a), .L_81_2726249e(decoder_trans_1_l_81_2726249e),
    .L_4_558283f2(decoder_trans_1_l_4_558283f2), .L_82_298ac22b(decoder_trans_1_l_82_298ac22b),
    .L_83_79a418b7(decoder_trans_1_l_83_79a418b7), .L_84_e79a1766(decoder_trans_1_l_84_e79a1766),
    .L_85_b2daf010(decoder_trans_1_l_85_b2daf010), .L_86_b98cc819(decoder_trans_1_l_86_b98cc819),
    .L_87_c637b311(decoder_trans_1_l_87_c637b311), .L_88_055bb603(decoder_trans_1_l_88_055bb603),
    .L_89_5d5fe4c7(decoder_trans_1_l_89_5d5fe4c7), .L_90_55afaa76(decoder_trans_1_l_90_55afaa76),
    .L_5_9518e519(decoder_trans_1_l_5_9518e519), .L_91_d03b9369(decoder_trans_1_l_91_d03b9369),
    .L_92_0cc1d36a(decoder_trans_1_l_92_0cc1d36a), .L_93_eaf60893(decoder_trans_1_l_93_eaf60893),
    .L_94_95326b03(decoder_trans_1_l_94_95326b03), .L_95_f060a0fd(decoder_trans_1_l_95_f060a0fd),
    .L_96_3d015798(decoder_trans_1_l_96_3d015798), .L_97_f3e813cd(decoder_trans_1_l_97_f3e813cd),
    .L_98_f4cee2ae(decoder_trans_1_l_98_f4cee2ae), .L_99_bb939962(decoder_trans_1_l_99_bb939962),
    .L_100_16b00339(decoder_trans_1_l_100_16b00339), .L_101_c09bb9ac(decoder_trans_1_l_101_c09bb9ac),
    .L_102_614a85bf(decoder_trans_1_l_102_614a85bf), .L_103_52940b9a(decoder_trans_1_l_103_52940b9a),
    .L_104_443c5ff0(decoder_trans_1_l_104_443c5ff0), .L_105_5ce959fd(decoder_trans_1_l_105_5ce959fd),
    .L_106_2a9581c6(decoder_trans_1_l_106_2a9581c6), .L_107_a96ffaba(decoder_trans_1_l_107_a96ffaba),
    .L_108_c205b5ff(decoder_trans_1_l_108_c205b5ff), .L_109_2fe88a94(decoder_trans_1_l_109_2fe88a94),
    .L_6_5b7e39b9(decoder_trans_1_l_6_5b7e39b9), .L_110_4cc555bd(decoder_trans_1_l_110_4cc555bd),
    .L_111_2b81c3c9(decoder_trans_1_l_111_2b81c3c9), .L_112_708a0f10(decoder_trans_1_l_112_708a0f10),
    .L_113_fbaa75ad(decoder_trans_1_l_113_fbaa75ad), .L_114_f9625e87(decoder_trans_1_l_114_f9625e87),
    .L_115_b1986fe2(decoder_trans_1_l_115_b1986fe2), .L_116_0ba24dc4(decoder_trans_1_l_116_0ba24dc4),
    .L_117_10a3c8b1(decoder_trans_1_l_117_10a3c8b1), .L_118_e0e8abfe(decoder_trans_1_l_118_e0e8abfe),
    .L_119_86db347d(decoder_trans_1_l_119_86db347d), .L_7_14ab2533(decoder_trans_1_l_7_14ab2533),
    .L_120_c53a083f(decoder_trans_1_l_120_c53a083f), .L_121_da158f44(decoder_trans_1_l_121_da158f44),
    .L_122_0e8f1988(decoder_trans_1_l_122_0e8f1988), .L_123_a8638cda(decoder_trans_1_l_123_a8638cda),
    .L_124_8d81fffd(decoder_trans_1_l_124_8d81fffd), .L_125_8f968e43(decoder_trans_1_l_125_8f968e43),
    .L_126_7e3003c6(decoder_trans_1_l_126_7e3003c6), .L_127_28942974(decoder_trans_1_l_127_28942974),
    .L_128_23d7200b(decoder_trans_1_l_128_23d7200b), .L_129_7b5e5edf(decoder_trans_1_l_129_7b5e5edf),
    .L_8_05eb4f56(decoder_trans_1_l_8_05eb4f56), .L_9_0082242d(decoder_trans_1_l_9_0082242d),
    .L_T5_89b31bc6(random_logic_1_l_t5_89b31bc6), .L_T4_d9b6e407(random_logic_1_l_t4_d9b6e407),
    .L_T3_3fe619b3(random_logic_1_l_t3_3fe619b3), .L_T2_37fe4d42(random_logic_1_l_t2_37fe4d42),
    .IR6(ir_1_ir6), .IR5(ir_1_ir5), .L_T0_5a901129(random_logic_1_l_t0_5a901129),
    .L_T1X_624de7e6(random_logic_1_l_t1x_624de7e6), .IR0(ir_1_ir0), .IR1(ir_1_ir1), .IR7(ir_1_ir7),
    .IR4(ir_1_ir4), .IR3(ir_1_ir3), .IR2(ir_1_ir2));
  RANDOM_LOGIC random_logic_1 (
    .L_D_OUT_7d61c6e7(random_logic_1_l_d_out_7d61c6e7), .L_C_OUT_f91ece9c(random_logic_1_l_c_out_f91ece9c),
    .L_N_OUT_10df9d15(random_logic_1_l_n_out_10df9d15), .L_Z_OUT_2813b2ba(random_logic_1_l_z_out_2813b2ba),
    .NDB_ADD_ee0a1870(random_logic_1_ndb_add_ee0a1870[0]),
    .DB_ADD_48d85b7e(random_logic_1_ndb_add_ee0a1870[1]),
    .L_0_ADD_81d17e61(random_logic_1_ndb_add_ee0a1870[2]),
    .SB_ADD_0eab26ac(random_logic_1_ndb_add_ee0a1870[3]),
    .ADL_ADD_e28b8a30(random_logic_1_ndb_add_ee0a1870[4]), .ANDS(random_logic_1_ndb_add_ee0a1870[8]),
    .EORS(random_logic_1_ndb_add_ee0a1870[9]), .ORS(random_logic_1_ndb_add_ee0a1870[10]),
    .L_ACIN_e173f520(random_logic_1_l_acin_e173f520[0]), .SUMS(random_logic_1_ndb_add_ee0a1870[12]),
    .L_DAA_82b80d94(random_logic_1_l_acin_e173f520[1]),
    .ADD_SB7_a8f4b77a(random_logic_1_ndb_add_ee0a1870[6]),
    .ADD_SB06_a3738230(random_logic_1_ndb_add_ee0a1870[5]),
    .ADD_ADL_3fac4345(random_logic_1_ndb_add_ee0a1870[7]),
    .L_DSA_ea96e89b(random_logic_1_l_acin_e173f520[2]), .SRS(random_logic_1_ndb_add_ee0a1870[11]),
    .DL_ADL_6c5e0116(random_logic_1_dl_adl_6c5e0116[0]), .DL_DB_69522204(random_logic_1_dl_adl_6c5e0116[1]),
    .DL_ADH_3839a3d0(random_logic_1_dl_adl_6c5e0116[2]),
    .ADH_ABH_8f72aca9(random_logic_1_adl_abl_5bea59e2[1]),
    .ADL_ABL_5bea59e2(random_logic_1_adl_abl_5bea59e2[0]), .SB_AC_b159eec5(random_logic_1_sb_ac_b159eec5[0]),
    .AC_SB_c49f602a(random_logic_1_sb_ac_b159eec5[1]), .L_0_ADH0_e340c71e(random_logic_1_sb_ac_b159eec5[5]),
    .L_0_ADH17_f181a8fa(random_logic_1_sb_ac_b159eec5[6]), .AC_DB_519ce409(random_logic_1_sb_ac_b159eec5[2]),
    .SB_DB_641efa5a(random_logic_1_sb_ac_b159eec5[3]), .SB_ADH_4f1456ff(random_logic_1_sb_ac_b159eec5[4]),
    .ADL_PCL_9a95c372(random_logic_1_adh_pch_61520abf[4]),
    .PCL_PCL_4f350f4d(random_logic_1_adh_pch_61520abf[5]),
    .PCH_ADH_ead93594(random_logic_1_adh_pch_61520abf[2]),
    .PCL_ADL_ee043dbc(random_logic_1_adh_pch_61520abf[6]),
    .PCH_DB_a81fefa0(random_logic_1_adh_pch_61520abf[3]),
    .L_0_ADL0_f8fabdab(random_logic_1_adl_abl_5bea59e2[2]),
    .PCL_DB_4172714e(random_logic_1_adh_pch_61520abf[7]),
    .ADH_PCH_61520abf(random_logic_1_adh_pch_61520abf[0]),
    .PCH_PCH_807b9fbd(random_logic_1_adh_pch_61520abf[1]), .TRESX(random_logic_1_tresx),
    .L_0_IR_c32b8001(random_logic_1_l_0_ir_c32b8001), .ENDS(random_logic_1_ends), .ENDX(random_logic_1_endx),
    .TRES1(random_logic_1_tres1), .T1(random_logic_1_t1),
    .L_0_ADL1_4e9a6ca8(random_logic_1_adl_abl_5bea59e2[3]), .L_T1X_624de7e6(random_logic_1_l_t1x_624de7e6),
    .RD(random_logic_1_rd), .R_W_47630a0a(random_logic_1_r_w_47630a0a),
    .L_1_PC_f2b91046(random_logic_1_adh_pch_61520abf[8]), .P_DB_42279b60(random_logic_1_p_db_42279b60),
    .IR5_I_e7eeeda5(random_logic_1_ir5_i_e7eeeda5), .IR5_C_8cbf3e52(random_logic_1_ir5_c_8cbf3e52),
    .IR5_D_ec89b364(random_logic_1_ir5_d_ec89b364), .L_0_V_f0a8dd83(random_logic_1_l_0_v_f0a8dd83),
    .DB7(random_logic_1_db0[7]), .ACR_C_5cb02b46(random_logic_1_acr_c_5cb02b46),
    .out_233(random_logic_1_db0[6]), .DBZ_Z_a7859eb1(random_logic_1_dbz_z_a7859eb1),
    .L_0_ADL2_2c4a79f4(random_logic_1_adl_abl_5bea59e2[4]), .out_234(random_logic_1_db0[5]),
    .DB_N_68ba26fc(random_logic_1_db_n_68ba26fc), .DB4(random_logic_1_db0[4]),
    .DB_P_37e5c1ba(random_logic_1_db_p_37e5c1ba), .out_236(random_logic_1_db0[3]),
    .DB_C_01ed158e(random_logic_1_db_c_01ed158e), .DB2(random_logic_1_db0[2]),
    .DB_V_92adf01b(random_logic_1_db_v_92adf01b), .out_238(random_logic_1_db0[1]),
    .DB0(random_logic_1_db0[0]), .Y_SB_d628d28f(random_logic_1_y_sb_d628d28f[0]),
    .L_T3_3fe619b3(random_logic_1_l_t3_3fe619b3), .L_T4_d9b6e407(random_logic_1_l_t4_d9b6e407),
    .L_T5_89b31bc6(random_logic_1_l_t5_89b31bc6), .WR(random_logic_1_wr), .FETCH(random_logic_1_fetch),
    .L_T0_5a901129(random_logic_1_l_t0_5a901129), .L_T2_37fe4d42(random_logic_1_l_t2_37fe4d42),
    .X_SB_222038db(random_logic_1_y_sb_d628d28f[2]), .SB_Y_9a33ae5e(random_logic_1_y_sb_d628d28f[1]),
    .SB_X_cf392641(random_logic_1_y_sb_d628d28f[3]), .S_SB_e37affed(random_logic_1_y_sb_d628d28f[7]),
    .S_ADL_07acd992(random_logic_1_y_sb_d628d28f[4]), .SB_S_4c94ee46(random_logic_1_y_sb_d628d28f[6]),
    .S_S_09f08a69(random_logic_1_y_sb_d628d28f[5]), .L_V_OUT_959779aa(random_logic_1_l_v_out_959779aa),
    .L_I_OUT_6792f219(random_logic_1_l_i_out_6792f219), .X25(decoder_trans_1_l_25_f5ad6aee),
    .X26(decoder_trans_1_l_26_ffeee2da), .X27(decoder_trans_1_l_27_6492a6f4),
    .X28(decoder_trans_1_l_28_647e552a), .X29(decoder_trans_1_l_29_1d3a3eb3),
    .X30(decoder_trans_1_l_30_3bf8f3d0), .X31(decoder_trans_1_l_31_e958c8e2),
    .X32(decoder_trans_1_l_32_7de83e69), .X33(decoder_trans_1_l_33_cae225fb),
    .X34(decoder_trans_1_l_34_97db28cb), .X35(decoder_trans_1_l_35_8b2262aa),
    .X36(decoder_trans_1_l_36_34609549), .X37(decoder_trans_1_l_37_acfb42d2),
    .X38(decoder_trans_1_l_38_43aa51c3), .X39(decoder_trans_1_l_39_c97a3f22),
    .X40(decoder_trans_1_l_40_1e6b68e0), .X41(decoder_trans_1_l_41_b24af141),
    .X42(decoder_trans_1_l_42_ae8bf3e0), .L_NMIP_021a4ca5(not_1_out), .RESP(d_latch_4_not_q),
    .L_IRQP_c24e1171(d_latch_1_not_q), .AVR(alu_1_avr), .ACR(alu_1_acr), .SO(SO),
    .X43(decoder_trans_1_l_43_fdaf143b), .X44(decoder_trans_1_l_44_bb416d4b),
    .X45(decoder_trans_1_l_45_e516ed8c), .X46(decoder_trans_1_l_46_6c10990a),
    .X47(decoder_trans_1_l_47_7c60183d), .X48(decoder_trans_1_l_48_330a6f3f),
    .X49(decoder_trans_1_l_49_f70f8148), .X50(decoder_trans_1_l_50_6b408103),
    .X51(decoder_trans_1_l_51_79fb832a), .X52(decoder_trans_1_l_52_253f2da2),
    .X53(decoder_trans_1_l_53_d08b6e35), .X54(decoder_trans_1_l_54_01afe50f),
    .X55(decoder_trans_1_l_55_73ecc214), .X56(decoder_trans_1_l_56_35bf93dd),
    .X57(decoder_trans_1_l_57_0f0af090), .X0(decoder_trans_1_l_0_090b2452),
    .X58(decoder_trans_1_l_58_4e7562c2), .X59(decoder_trans_1_l_59_d4e3d539),
    .X60(decoder_trans_1_l_60_8c46ae22), .X61(decoder_trans_1_l_61_ef440803),
    .X62(decoder_trans_1_l_62_1470bf03), .X63(decoder_trans_1_l_63_0a5e7e38),
    .X64(decoder_trans_1_l_64_e6cb4ce5), .X65(decoder_trans_1_l_65_6a42b4dc),
    .X66(decoder_trans_1_l_66_3306dbdf), .X1(decoder_trans_1_l_1_28cbbb7d),
    .X67(decoder_trans_1_l_67_7ef59d0e), .X68(decoder_trans_1_l_68_820561b0),
    .X69(decoder_trans_1_l_69_cbdecb8a), .X70(decoder_trans_1_l_70_099188dc),
    .X71(decoder_trans_1_l_71_facae7ec), .X72(decoder_trans_1_l_72_92460769),
    .X73(decoder_trans_1_l_73_3c19a6e4), .X74(decoder_trans_1_l_74_b252c222),
    .X75(decoder_trans_1_l_75_7b13a6b0), .X2(decoder_trans_1_l_2_143403ae),
    .X76(decoder_trans_1_l_76_ea80c3c2), .X77(decoder_trans_1_l_77_f96dcb28),
    .X78(decoder_trans_1_l_78_8a0d457e), .X79(decoder_trans_1_l_79_7d8df45e),
    .X80(decoder_trans_1_l_80_053c0a7a), .X81(decoder_trans_1_l_81_2726249e),
    .X82(decoder_trans_1_l_82_298ac22b), .X83(decoder_trans_1_l_83_79a418b7),
    .X84(decoder_trans_1_l_84_e79a1766), .X3(decoder_trans_1_l_3_39a566ac),
    .X85(decoder_trans_1_l_85_b2daf010), .X86(decoder_trans_1_l_86_b98cc819),
    .X87(decoder_trans_1_l_87_c637b311), .X88(decoder_trans_1_l_88_055bb603),
    .X89(decoder_trans_1_l_89_5d5fe4c7), .X90(decoder_trans_1_l_90_55afaa76),
    .X91(decoder_trans_1_l_91_d03b9369), .X92(decoder_trans_1_l_92_0cc1d36a),
    .X93(decoder_trans_1_l_93_eaf60893), .X4(decoder_trans_1_l_4_558283f2),
    .X94(decoder_trans_1_l_94_95326b03), .X95(decoder_trans_1_l_95_f060a0fd),
    .X96(decoder_trans_1_l_96_3d015798), .X97(decoder_trans_1_l_97_f3e813cd),
    .X98(decoder_trans_1_l_98_f4cee2ae), .X99(decoder_trans_1_l_99_bb939962),
    .X100(decoder_trans_1_l_100_16b00339), .X101(decoder_trans_1_l_101_c09bb9ac),
    .X102(decoder_trans_1_l_102_614a85bf), .X5(decoder_trans_1_l_5_9518e519),
    .X103(decoder_trans_1_l_103_52940b9a), .X104(decoder_trans_1_l_104_443c5ff0),
    .X105(decoder_trans_1_l_105_5ce959fd), .X106(decoder_trans_1_l_106_2a9581c6),
    .X107(decoder_trans_1_l_107_a96ffaba), .X108(decoder_trans_1_l_108_c205b5ff),
    .X109(decoder_trans_1_l_109_2fe88a94), .X110(decoder_trans_1_l_110_4cc555bd),
    .X111(decoder_trans_1_l_111_2b81c3c9), .X6(decoder_trans_1_l_6_5b7e39b9),
    .X112(decoder_trans_1_l_112_708a0f10), .X113(decoder_trans_1_l_113_fbaa75ad),
    .X114(decoder_trans_1_l_114_f9625e87), .X115(decoder_trans_1_l_115_b1986fe2),
    .X116(decoder_trans_1_l_116_0ba24dc4), .X117(decoder_trans_1_l_117_10a3c8b1),
    .X118(decoder_trans_1_l_118_e0e8abfe), .X119(decoder_trans_1_l_119_86db347d),
    .X120(decoder_trans_1_l_120_c53a083f), .X7(decoder_trans_1_l_7_14ab2533),
    .X121(decoder_trans_1_l_121_da158f44), .X122(decoder_trans_1_l_122_0e8f1988),
    .X123(decoder_trans_1_l_123_a8638cda), .X124(decoder_trans_1_l_124_8d81fffd),
    .X125(decoder_trans_1_l_125_8f968e43), .X126(decoder_trans_1_l_126_7e3003c6),
    .X127(decoder_trans_1_l_127_28942974), .X128(decoder_trans_1_l_128_23d7200b),
    .X129(decoder_trans_1_l_129_7b5e5edf), .X8(decoder_trans_1_l_8_05eb4f56), .in_143(random_logic_1_db0[7]),
    .DB6(random_logic_1_db0[6]), .DB5(random_logic_1_db0[5]), .in_146(random_logic_1_db0[4]),
    .DB3(random_logic_1_db0[3]), .X9(decoder_trans_1_l_9_0082242d), .in_148(random_logic_1_db0[2]),
    .PHI2(PHI2), .L_IR5_9e15d54c(not_3_out), .PHI1(PHI1),
    .L_TWOCYCLE_54b4f369(predecode_1_l_twocycle_54b4f369),
    .L_IMPLIED_b029c4af(predecode_1_l_implied_b029c4af), .RDY(d_latch_3_not_q), .DB1(random_logic_1_db0[1]),
    .in_150(random_logic_1_db0[0]), .X10(decoder_trans_1_l_10_57b0d741), .X11(decoder_trans_1_l_11_aa2e7fa3),
    .X12(decoder_trans_1_l_12_85a3418f), .X13(decoder_trans_1_l_13_587da886),
    .X14(decoder_trans_1_l_14_4f483598), .X15(decoder_trans_1_l_15_5dad5732),
    .X16(decoder_trans_1_l_16_c7396848), .X17(decoder_trans_1_l_17_0f5278c7),
    .X18(decoder_trans_1_l_18_4ab117a9), .X19(decoder_trans_1_l_19_e094c090),
    .X20(decoder_trans_1_l_20_adeacd1b), .X21(decoder_trans_1_l_21_ada5c31c),
    .X22(decoder_trans_1_l_22_f545d19e), .X23(decoder_trans_1_l_23_d0835dd9),
    .X24(decoder_trans_1_l_24_b6efc2f4));
  not not_1 (not_1_out, d_ff_1_qn);
  ABL abl_1 (
    .A0(A0), .A1(A1), .A2(A2), .A3(A3), .A4(A4), .A5(A5), .A6(A6), .A7(A7),
    .ADL_ABL(random_logic_1_adl_abl_5bea59e2[0]), .L_0_ADL0(random_logic_1_adl_abl_5bea59e2[2]),
    .L_0_ADL1(random_logic_1_adl_abl_5bea59e2[3]), .L_0_ADL2(random_logic_1_adl_abl_5bea59e2[4]),
    .ADL0(regs_1_adl0[0]), .PHI1(PHI1), .ADL1(regs_1_adl0[1]), .ADL2(regs_1_adl0[2]), .ADL3(regs_1_adl0[3]),
    .ADL4(regs_1_adl0[4]), .ADL5(regs_1_adl0[5]), .ADL6(regs_1_adl0[6]), .ADL7(regs_1_adl0[7]), .PHI2(PHI2));
  ABH abh_1 (
    .A8(A8), .A9(A9), .A10(A10), .A11(A11), .A12(A12), .A13(A13), .A14(A14), .A15(A15), .ADH0(alu_1_adh0[0]),
    .ADH1(alu_1_adh0[1]), .ADH2(alu_1_adh0[2]), .PHI1(PHI1), .ADH3(alu_1_adh0[3]), .ADH4(alu_1_adh0[4]),
    .ADH5(alu_1_adh0[5]), .ADH6(alu_1_adh0[6]), .ADH7(alu_1_adh0[7]), .PHI2(PHI2),
    .ADH_ABH_8f72aca9(random_logic_1_adl_abl_5bea59e2[1]));
  D_Flip_Flop #(.trigger("high")) d_ff_2 (.D(n_IRQ), .clk(PHI2), .Qn(d_ff_2_qn));  // open: Q, preset, reset
  D_Latch d_latch_1 (.NOT_Q(d_latch_1_not_q), .D(d_ff_2_qn), .EN(PHI1));  // open: Q
  Register #(.trigger("high")) X (.D(regs_1_x_debug), .en(1'b1), .clk(1'b1));  // open: Q, clr
  REGS regs_1 (
    .S_Debug(regs_1_s_debug), .SB1_Out(regs_1_sb0_out[1]), .SB2_Out(regs_1_sb0_out[2]),
    .SB3_Out(regs_1_sb0_out[3]), .SB4_Out(regs_1_sb0_out[4]), .SB5_Out(regs_1_sb0_out[5]),
    .SB6_Out(regs_1_sb0_out[6]), .SB7_Out(regs_1_sb0_out[7]), .ADL0(regs_1_adl0[0]), .ADL1(regs_1_adl0[1]),
    .ADL2(regs_1_adl0[2]), .ADL3(regs_1_adl0[3]), .ADL4(regs_1_adl0[4]), .ADL5(regs_1_adl0[5]),
    .ADL6(regs_1_adl0[6]), .ADL7(regs_1_adl0[7]), .SB0_Out(regs_1_sb0_out[0]), .Y_Debug(regs_1_y_debug),
    .X_Debug(regs_1_x_debug), .Y_SB(random_logic_1_y_sb_d628d28f[0]), .SB_Y(random_logic_1_y_sb_d628d28f[1]),
    .X_SB(random_logic_1_y_sb_d628d28f[2]), .SB_X(random_logic_1_y_sb_d628d28f[3]),
    .S_ADL(random_logic_1_y_sb_d628d28f[4]), .S_S(random_logic_1_y_sb_d628d28f[5]),
    .SB_S(random_logic_1_y_sb_d628d28f[6]), .S_SB(random_logic_1_y_sb_d628d28f[7]),
    .SB0_In(regs_1_sb0_out[0]), .SB1_In(regs_1_sb0_out[1]), .SB2_In(regs_1_sb0_out[2]),
    .SB3_In(regs_1_sb0_out[3]), .SB4_In(regs_1_sb0_out[4]), .SB5_In(regs_1_sb0_out[5]),
    .SB6_In(regs_1_sb0_out[6]), .PHI2(PHI2), .SB7_In(regs_1_sb0_out[7]));
  Register #(.trigger("high")) Y (.D(regs_1_y_debug), .en(1'b1), .clk(1'b1));  // open: Q, clr
  Register #(.trigger("high")) S (.D(regs_1_s_debug), .en(1'b1), .clk(1'b1));  // open: Q, clr
  not not_2 (not_2_out, RDY);
  Register #(.trigger("high")) AI (.D(alu_1_ai_debug), .en(1'b1), .clk(1'b1));  // open: Q, clr
  D_Latch d_latch_2 (.NOT_Q(d_latch_2_not_q), .D(not_2_out), .EN(PHI2));  // open: Q
  ALU alu_1 (
    .SB4(regs_1_sb0_out[4]), .out_75(regs_1_sb0_out[5]), .out_79(regs_1_sb0_out[6]), .SB7(regs_1_sb0_out[7]),
    .out_55(regs_1_sb0_out[0]), .SB1(regs_1_sb0_out[1]), .out_63(regs_1_sb0_out[2]),
    .out_67(regs_1_sb0_out[3]), .DB4(random_logic_1_db0[4]), .out_76(random_logic_1_db0[5]),
    .out_80(random_logic_1_db0[6]), .DB7(random_logic_1_db0[7]), .DB0(random_logic_1_db0[0]),
    .out_60(random_logic_1_db0[1]), .DB2(random_logic_1_db0[2]), .DB3(random_logic_1_db0[3]),
    .ADL4(regs_1_adl0[4]), .out_77(regs_1_adl0[5]), .ADL6(regs_1_adl0[6]), .out_85(regs_1_adl0[7]),
    .out_57(regs_1_adl0[0]), .out_61(regs_1_adl0[1]), .ADL2(regs_1_adl0[2]), .out_69(regs_1_adl0[3]),
    .AC_Debug(alu_1_ac_debug), .ADH4(alu_1_adh0[4]), .ADH5(alu_1_adh0[5]), .ADH6(alu_1_adh0[6]),
    .ADH7(alu_1_adh0[7]), .ADH0(alu_1_adh0[0]), .ADH1(alu_1_adh0[1]), .ADH2(alu_1_adh0[2]),
    .ADH3(alu_1_adh0[3]), .AVR(alu_1_avr), .ACR(alu_1_acr), .AI_Debug(alu_1_ai_debug),
    .BI_Debug(alu_1_bi_debug), .ADD_Debug(alu_1_add_debug), .in_37(regs_1_sb0_out[4]),
    .SB5(regs_1_sb0_out[5]), .SB6(regs_1_sb0_out[6]), .NDB_ADD_ee0a1870(random_logic_1_ndb_add_ee0a1870[0]),
    .in_46(regs_1_sb0_out[7]), .DB_ADD_48d85b7e(random_logic_1_ndb_add_ee0a1870[1]),
    .L_0_ADD_81d17e61(random_logic_1_ndb_add_ee0a1870[2]), .PHI2(PHI2),
    .SB_ADD_0eab26ac(random_logic_1_ndb_add_ee0a1870[3]),
    .ADL_ADD_e28b8a30(random_logic_1_ndb_add_ee0a1870[4]),
    .ADD_SB06_a3738230(random_logic_1_ndb_add_ee0a1870[5]),
    .ADD_SB7_a8f4b77a(random_logic_1_ndb_add_ee0a1870[6]),
    .ADD_ADL_3fac4345(random_logic_1_ndb_add_ee0a1870[7]), .ANDS(random_logic_1_ndb_add_ee0a1870[8]),
    .EORS(random_logic_1_ndb_add_ee0a1870[9]), .ORS(random_logic_1_ndb_add_ee0a1870[10]),
    .SRS(random_logic_1_ndb_add_ee0a1870[11]), .SUMS(random_logic_1_ndb_add_ee0a1870[12]),
    .SB_AC_b159eec5(random_logic_1_sb_ac_b159eec5[0]), .AC_SB_c49f602a(random_logic_1_sb_ac_b159eec5[1]),
    .AC_DB_519ce409(random_logic_1_sb_ac_b159eec5[2]), .SB_DB_641efa5a(random_logic_1_sb_ac_b159eec5[3]),
    .SB_ADH_4f1456ff(random_logic_1_sb_ac_b159eec5[4]), .L_0_ADH0_e340c71e(random_logic_1_sb_ac_b159eec5[5]),
    .L_0_ADH17_f181a8fa(random_logic_1_sb_ac_b159eec5[6]),
    .L_ACIN_e173f520(random_logic_1_l_acin_e173f520[0]), .L_DAA_82b80d94(random_logic_1_l_acin_e173f520[1]),
    .L_DSA_ea96e89b(random_logic_1_l_acin_e173f520[2]), .SB0(regs_1_sb0_out[0]), .in_28(regs_1_sb0_out[1]),
    .SB2(regs_1_sb0_out[2]), .SB3(regs_1_sb0_out[3]), .in_38(random_logic_1_db0[4]),
    .DB5(random_logic_1_db0[5]), .DB6(random_logic_1_db0[6]), .in_47(random_logic_1_db0[7]),
    .in_26(random_logic_1_db0[0]), .DB1(random_logic_1_db0[1]), .in_32(random_logic_1_db0[2]),
    .in_35(random_logic_1_db0[3]), .in_39(regs_1_adl0[4]), .ADL5(regs_1_adl0[5]), .in_45(regs_1_adl0[6]),
    .ADL7(regs_1_adl0[7]), .ADL0(regs_1_adl0[0]), .ADL1(regs_1_adl0[1]), .in_33(regs_1_adl0[2]),
    .ADL3(regs_1_adl0[3]));
  Register #(.trigger("high")) BI (.D(alu_1_bi_debug), .en(1'b1), .clk(1'b1));  // open: Q, clr
  D_Flip_Flop #(.trigger("high")) d_ff_3 (.D(n_RES), .clk(PHI2), .Q(d_ff_3_q));  // open: Qn, preset, reset
  D_Latch d_latch_3 (.NOT_Q(d_latch_3_not_q), .D(d_latch_2_not_q), .EN(PHI1));  // open: Q
  Register #(.trigger("high")) ADD (.D(alu_1_add_debug), .en(1'b1), .clk(1'b1));  // open: Q, clr
  Register #(.trigger("high")) AC (.D(alu_1_ac_debug), .en(1'b1), .clk(1'b1));  // open: Q, clr
  D_Latch d_latch_4 (.NOT_Q(d_latch_4_not_q), .D(d_ff_3_q), .EN(PHI1));  // open: Q
  PC pc_1 (
    .DB2(random_logic_1_db0[2]), .DB3(random_logic_1_db0[3]), .DB4(random_logic_1_db0[4]),
    .DB5(random_logic_1_db0[5]), .DB6(random_logic_1_db0[6]), .DB7(random_logic_1_db0[7]),
    .ADL0(regs_1_adl0[0]), .out_36(regs_1_adl0[1]), .out_37(regs_1_adl0[2]), .out_38(regs_1_adl0[3]),
    .out_39(regs_1_adl0[4]), .out_40(regs_1_adl0[5]), .ADL6(regs_1_adl0[6]), .DB0(random_logic_1_db0[0]),
    .out_42(regs_1_adl0[7]), .ADH0(alu_1_adh0[0]), .ADH1(alu_1_adh0[1]), .ADH2(alu_1_adh0[2]),
    .out_46(alu_1_adh0[3]), .ADH4(alu_1_adh0[4]), .ADH5(alu_1_adh0[5]), .ADH6(alu_1_adh0[6]),
    .ADH7(alu_1_adh0[7]), .DB1(random_logic_1_db0[1]), .PC_Debug(pc_1_pc_debug), .PCS_Debug(pc_1_pcs_debug),
    .ADL_PCL_9a95c372(random_logic_1_adh_pch_61520abf[4]),
    .PCL_PCL_4f350f4d(random_logic_1_adh_pch_61520abf[5]),
    .PCL_ADL_ee043dbc(random_logic_1_adh_pch_61520abf[6]),
    .PCL_DB_4172714e(random_logic_1_adh_pch_61520abf[7]),
    .ADH_PCH_61520abf(random_logic_1_adh_pch_61520abf[0]),
    .PCH_PCH_807b9fbd(random_logic_1_adh_pch_61520abf[1]),
    .PCH_ADH_ead93594(random_logic_1_adh_pch_61520abf[2]),
    .PCH_DB_a81fefa0(random_logic_1_adh_pch_61520abf[3]),
    .L_1_PC_f2b91046(random_logic_1_adh_pch_61520abf[8]), .PHI2(PHI2), .in_11(regs_1_adl0[0]),
    .ADL1(regs_1_adl0[1]), .ADL2(regs_1_adl0[2]), .ADL3(regs_1_adl0[3]), .ADL4(regs_1_adl0[4]),
    .ADL5(regs_1_adl0[5]), .in_17(regs_1_adl0[6]), .ADL7(regs_1_adl0[7]), .in_19(alu_1_adh0[0]),
    .in_20(alu_1_adh0[1]), .in_21(alu_1_adh0[2]), .ADH3(alu_1_adh0[3]), .in_23(alu_1_adh0[4]),
    .in_24(alu_1_adh0[5]), .in_25(alu_1_adh0[6]), .in_26(alu_1_adh0[7]));
  Register #(.trigger("high"), .width(16)) PC_2 (.D(pc_1_pc_debug), .en(1'b1), .clk(1'b1));  // open: Q, clr
  Register #(.trigger("high"), .width(16)) PCS (.D(pc_1_pcs_debug), .en(1'b1), .clk(1'b1));  // open: Q, clr
  CLOCKGEN clockgen_1 (.PHI2(PHI2), .PHI1(PHI1), .PHI0(PHI0_out));
  Clock PHI0 (.out(PHI0_out));
  not not_3 (not_3_out, ir_1_ir5);
  DL dl_1 (
    .D6(D6_OUT), .D7(D7_OUT), .out_25(random_logic_1_db0[2]), .DB3(random_logic_1_db0[3]),
    .DB4(random_logic_1_db0[4]), .out_28(random_logic_1_db0[5]), .out_29(random_logic_1_db0[6]),
    .out_30(random_logic_1_db0[7]), .ADL0(regs_1_adl0[0]), .ADL1(regs_1_adl0[1]), .ADL2(regs_1_adl0[2]),
    .ADL3(regs_1_adl0[3]), .ADL4(regs_1_adl0[4]), .ADL5(regs_1_adl0[5]), .ADL6(regs_1_adl0[6]),
    .ADL7(regs_1_adl0[7]), .ADH0(alu_1_adh0[0]), .DB0(random_logic_1_db0[0]), .ADH1(alu_1_adh0[1]),
    .ADH2(alu_1_adh0[2]), .ADH3(alu_1_adh0[3]), .ADH4(alu_1_adh0[4]), .ADH5(alu_1_adh0[5]),
    .ADH6(alu_1_adh0[6]), .ADH7(alu_1_adh0[7]), .D0(D0_OUT), .out_48(D1_OUT), .D2(D2_OUT),
    .DB1(random_logic_1_db0[1]), .out_50(D3_OUT), .out_51(D4_OUT), .D5(D5_OUT), .DL_Debug(dl_1_dl_debug),
    .DOR_Debug(dl_1_dor_debug), .WR(random_logic_1_wr), .DL_ADL_6c5e0116(random_logic_1_dl_adl_6c5e0116[0]),
    .DL_ADH_3839a3d0(random_logic_1_dl_adl_6c5e0116[2]), .DL_DB_69522204(random_logic_1_dl_adl_6c5e0116[1]),
    .in_7(random_logic_1_db0[0]), .in_8(random_logic_1_db0[1]), .DB2(random_logic_1_db0[2]),
    .in_10(random_logic_1_db0[3]), .in_11(random_logic_1_db0[4]), .DB5(random_logic_1_db0[5]), .PHI1(PHI1),
    .DB6(random_logic_1_db0[6]), .DB7(random_logic_1_db0[7]), .in_15(D0_IN), .D1(D1_IN), .in_17(D2_IN),
    .D3(D3_IN), .D4(D4_IN), .PHI2(PHI2), .in_20(D5_IN), .in_21(D6_IN), .in_22(D7_IN));
  Register #(.trigger("high")) DL_2 (.D(dl_1_dl_debug), .en(1'b1), .clk(1'b1));  // open: Q, clr
  D_Latch RWLatch (.NOT_Q(R_W), .D(random_logic_1_wr), .EN(PHI1));  // open: Q
  IR ir_1 (
    .IR0(ir_1_ir0), .IR1(ir_1_ir1), .IR2(ir_1_ir2), .IR3(ir_1_ir3), .IR4(ir_1_ir4), .IR5(ir_1_ir5),
    .IR6(ir_1_ir6), .IR7(ir_1_ir7), .L_in0_dea3fa9c(predecode_1_l_pd0_ff4f5362),
    .L_in1_3405e045(predecode_1_l_pd1_2bbb5f50), .L_in2_d55e1188(predecode_1_l_pd2_b780aebe),
    .L_in3_e63baf83(predecode_1_l_pd3_595d30b7), .L_in4_b1b51af8(predecode_1_l_pd4_d7b0250f),
    .L_in5_af1dd408(predecode_1_l_pd5_1b763385), .L_in6_328834da(predecode_1_l_pd6_cacfa412),
    .L_in7_b8770e13(predecode_1_l_pd7_1b7e0f3f), .FETCH(random_logic_1_fetch), .PHI1(PHI1));
  Register #(.trigger("high")) DOR (.D(dl_1_dor_debug), .en(1'b1), .clk(1'b1));  // open: Q, clr
  PREDECODE predecode_1 (
    .L_TWOCYCLE_54b4f369(predecode_1_l_twocycle_54b4f369),
    .L_IMPLIED_b029c4af(predecode_1_l_implied_b029c4af), .L_PD0_ff4f5362(predecode_1_l_pd0_ff4f5362),
    .L_PD1_2bbb5f50(predecode_1_l_pd1_2bbb5f50), .L_PD2_b780aebe(predecode_1_l_pd2_b780aebe),
    .L_PD3_595d30b7(predecode_1_l_pd3_595d30b7), .L_PD4_d7b0250f(predecode_1_l_pd4_d7b0250f),
    .L_PD5_1b763385(predecode_1_l_pd5_1b763385), .L_PD6_cacfa412(predecode_1_l_pd6_cacfa412),
    .L_PD7_1b7e0f3f(predecode_1_l_pd7_1b7e0f3f), .D0(D0_IN), .PHI2(PHI2), .D1(D1_IN), .D2(D2_IN), .D3(D3_IN),
    .D4(D4_IN), .D5(D5_IN), .L_0_IR_c32b8001(random_logic_1_l_0_ir_c32b8001), .D6(D6_IN), .D7(D7_IN));

  // Notes on the sheet:
  //   PHI2
  //   PHI1
  //   PHI1
  //   PHI2
  //   T1
  //   The pin layout corresponds to the real chip
  //   /NMIP
  //   ADH
  //   ADL
  //   /IRQP
  //   DB
  //   SB
  //   DEBUG
  //   /RDY
  //   DEBUG
  //   RESP
  //   DEBUG
  //   PHI2
  //   PHI1
  //   WR
  //   DEBUG
  //   PHI1
  //   PHI2
endmodule

module CLOCKGEN (
  input  PHI0,
  output PHI2,
  output PHI1
);

  wire not_1_out;

  not not_1 (not_1_out, PHI0);
  not not_2 (PHI2, not_1_out);
  not not_3 (PHI1, PHI0);
endmodule

module IR (
  input  FETCH,
  input  PHI1,
  input  L_in0_dea3fa9c,
  input  L_in1_3405e045,
  input  L_in2_d55e1188,
  input  L_in3_e63baf83,
  input  L_in4_b1b51af8,
  input  L_in5_af1dd408,
  input  L_in6_328834da,
  input  L_in7_b8770e13,
  output IR0,
  output IR1,
  output IR2,
  output IR3,
  output IR4,
  output IR5,
  output IR6,
  output IR7
);

  wire and1_out;

  and and1 (and1_out, FETCH, PHI1);
  D_Latch d_latch_1 (.NOT_Q(IR0), .D(L_in0_dea3fa9c), .EN(and1_out));  // open: Q
  D_Latch d_latch_2 (.NOT_Q(IR1), .D(L_in1_3405e045), .EN(and1_out));  // open: Q
  D_Latch d_latch_3 (.NOT_Q(IR2), .D(L_in2_d55e1188), .EN(and1_out));  // open: Q
  D_Latch d_latch_4 (.NOT_Q(IR3), .D(L_in3_e63baf83), .EN(and1_out));  // open: Q
  D_Latch d_latch_5 (.NOT_Q(IR4), .D(L_in4_b1b51af8), .EN(and1_out));  // open: Q
  D_Latch d_latch_6 (.NOT_Q(IR5), .D(L_in5_af1dd408), .EN(and1_out));  // open: Q
  D_Latch d_latch_7 (.NOT_Q(IR6), .D(L_in6_328834da), .EN(and1_out));  // open: Q
  D_Latch d_latch_8 (.NOT_Q(IR7), .D(L_in7_b8770e13), .EN(and1_out));  // open: Q
endmodule
// DECODER
module DECODER_TRANS (
  input  L_T5_89b31bc6,
  input  L_T4_d9b6e407,
  input  L_T3_3fe619b3,
  input  L_T2_37fe4d42,
  input  IR0,
  input  IR1,
  input  IR7,
  input  IR4,
  input  IR3,
  input  IR2,
  input  IR6,
  input  IR5,
  input  L_T0_5a901129,
  input  L_T1X_624de7e6,
  output L_0_090b2452,
  output L_1_28cbbb7d,
  output L_2_143403ae,
  output L_3_39a566ac,
  output L_4_558283f2,
  output L_5_9518e519,
  output L_6_5b7e39b9,
  output L_7_14ab2533,
  output L_8_05eb4f56,
  output L_9_0082242d,
  output L_10_57b0d741,
  output L_11_aa2e7fa3,
  output L_12_85a3418f,
  output L_13_587da886,
  output L_14_4f483598,
  output L_15_5dad5732,
  output L_16_c7396848,
  output L_17_0f5278c7,
  output L_18_4ab117a9,
  output L_19_e094c090,
  output L_20_adeacd1b,
  output L_21_ada5c31c,
  output L_22_f545d19e,
  output L_23_d0835dd9,
  output L_24_b6efc2f4,
  output L_25_f5ad6aee,
  output L_26_ffeee2da,
  output L_27_6492a6f4,
  output L_28_647e552a,
  output L_29_1d3a3eb3,
  output L_30_3bf8f3d0,
  output L_31_e958c8e2,
  output L_32_7de83e69,
  output L_33_cae225fb,
  output L_34_97db28cb,
  output L_35_8b2262aa,
  output L_36_34609549,
  output L_37_acfb42d2,
  output L_38_43aa51c3,
  output L_39_c97a3f22,
  output L_40_1e6b68e0,
  output L_41_b24af141,
  output L_42_ae8bf3e0,
  output L_43_fdaf143b,
  output L_44_bb416d4b,
  output L_45_e516ed8c,
  output L_46_6c10990a,
  output L_47_7c60183d,
  output L_48_330a6f3f,
  output L_49_f70f8148,
  output L_50_6b408103,
  output L_51_79fb832a,
  output L_52_253f2da2,
  output L_53_d08b6e35,
  output L_54_01afe50f,
  output L_55_73ecc214,
  output L_56_35bf93dd,
  output L_57_0f0af090,
  output L_58_4e7562c2,
  output L_59_d4e3d539,
  output L_60_8c46ae22,
  output L_61_ef440803,
  output L_62_1470bf03,
  output L_63_0a5e7e38,
  output L_64_e6cb4ce5,
  output L_65_6a42b4dc,
  output L_66_3306dbdf,
  output L_67_7ef59d0e,
  output L_68_820561b0,
  output L_69_cbdecb8a,
  output L_70_099188dc,
  output L_71_facae7ec,
  output L_72_92460769,
  output L_73_3c19a6e4,
  output L_74_b252c222,
  output L_75_7b13a6b0,
  output L_76_ea80c3c2,
  output L_77_f96dcb28,
  output L_78_8a0d457e,
  output L_79_7d8df45e,
  output L_80_053c0a7a,
  output L_81_2726249e,
  output L_82_298ac22b,
  output L_83_79a418b7,
  output L_84_e79a1766,
  output L_85_b2daf010,
  output L_86_b98cc819,
  output L_87_c637b311,
  output L_88_055bb603,
  output L_89_5d5fe4c7,
  output L_90_55afaa76,
  output L_91_d03b9369,
  output L_92_0cc1d36a,
  output L_93_eaf60893,
  output L_94_95326b03,
  output L_95_f060a0fd,
  output L_96_3d015798,
  output L_97_f3e813cd,
  output L_98_f4cee2ae,
  output L_99_bb939962,
  output L_100_16b00339,
  output L_101_c09bb9ac,
  output L_102_614a85bf,
  output L_103_52940b9a,
  output L_104_443c5ff0,
  output L_105_5ce959fd,
  output L_106_2a9581c6,
  output L_107_a96ffaba,
  output L_108_c205b5ff,
  output L_109_2fe88a94,
  output L_110_4cc555bd,
  output L_111_2b81c3c9,
  output L_112_708a0f10,
  output L_113_fbaa75ad,
  output L_114_f9625e87,
  output L_115_b1986fe2,
  output L_116_0ba24dc4,
  output L_117_10a3c8b1,
  output L_118_e0e8abfe,
  output L_119_86db347d,
  output L_120_c53a083f,
  output L_121_da158f44,
  output L_122_0e8f1988,
  output L_123_a8638cda,
  output L_124_8d81fffd,
  output L_125_8f968e43,
  output L_126_7e3003c6,
  output L_127_28942974,
  output L_128_23d7200b,
  output L_129_7b5e5edf
);

  wire not_1_out, not_2_out, not_3_out, not_4_out, not_5_out, not_6_out, not_7_out, not_8_out, or_1_out;

  not not_1 (not_1_out, IR1);
  or or_1 (or_1_out, IR0, IR1);
  not not_2 (not_2_out, IR0);
  not not_3 (not_3_out, IR7);
  not not_4 (not_4_out, IR4);
  not not_5 (not_5_out, IR3);
  not not_6 (not_6_out, IR2);
  not not_7 (not_7_out, IR6);
  not not_8 (not_8_out, IR5);
  Pull_Resistor #(.pull(1)) pull_resistor_1 (.node(L_0_090b2452));
  Pull_Resistor #(.pull(1)) pull_resistor_2 (.node(L_1_28cbbb7d));
  Transistor #(.\type ("n")) transistor_1 (.in(1'b0), .out(L_1_28cbbb7d), .gate(L_T3_3fe619b3));
  Transistor #(.\type ("n")) transistor_2 (.in(1'b0), .out(L_0_090b2452), .gate(or_1_out));
  Transistor #(.\type ("n")) transistor_3 (.in(1'b0), .out(L_1_28cbbb7d), .gate(not_2_out));
  Transistor #(.\type ("n")) transistor_4 (.in(1'b0), .out(L_0_090b2452), .gate(not_3_out));
  Transistor #(.\type ("n")) transistor_5 (.in(1'b0), .out(L_0_090b2452), .gate(not_4_out));
  Transistor #(.\type ("n")) transistor_6 (.in(1'b0), .out(L_1_28cbbb7d), .gate(not_4_out));
  Transistor #(.\type ("n")) transistor_7 (.in(1'b0), .out(L_1_28cbbb7d), .gate(IR3));
  Transistor #(.\type ("n")) transistor_8 (.in(1'b0), .out(L_1_28cbbb7d), .gate(IR2));
  Transistor #(.\type ("n")) transistor_9 (.in(1'b0), .out(L_0_090b2452), .gate(not_6_out));
  Transistor #(.\type ("n")) transistor_10 (.in(1'b0), .out(L_0_090b2452), .gate(IR6));
  Transistor #(.\type ("n")) transistor_11 (.in(1'b0), .out(L_0_090b2452), .gate(IR5));
  Pull_Resistor #(.pull(1)) pull_resistor_3 (.node(L_2_143403ae));
  Transistor #(.\type ("n")) transistor_12 (.in(1'b0), .out(L_2_143403ae), .gate(L_T2_37fe4d42));
  Transistor #(.\type ("n")) transistor_13 (.in(1'b0), .out(L_2_143403ae), .gate(not_2_out));
  Transistor #(.\type ("n")) transistor_14 (.in(1'b0), .out(L_2_143403ae), .gate(not_4_out));
  Transistor #(.\type ("n")) transistor_15 (.in(1'b0), .out(L_2_143403ae), .gate(not_5_out));
  Transistor #(.\type ("n")) transistor_16 (.in(1'b0), .out(L_2_143403ae), .gate(IR2));
  Pull_Resistor #(.pull(1)) pull_resistor_4 (.node(L_3_39a566ac));
  Transistor #(.\type ("n")) transistor_17 (.in(1'b0), .out(L_3_39a566ac), .gate(or_1_out));
  Transistor #(.\type ("n")) transistor_18 (.in(1'b0), .out(L_3_39a566ac), .gate(not_3_out));
  Transistor #(.\type ("n")) transistor_19 (.in(1'b0), .out(L_3_39a566ac), .gate(IR4));
  Transistor #(.\type ("n")) transistor_20 (.in(1'b0), .out(L_3_39a566ac), .gate(not_5_out));
  Transistor #(.\type ("n")) transistor_21 (.in(1'b0), .out(L_3_39a566ac), .gate(IR2));
  Transistor #(.\type ("n")) transistor_22 (.in(1'b0), .out(L_3_39a566ac), .gate(IR5));
  Transistor #(.\type ("n")) transistor_23 (.in(1'b0), .out(L_3_39a566ac), .gate(L_T0_5a901129));
  Pull_Resistor #(.pull(1)) pull_resistor_5 (.node(L_4_558283f2));
  Pull_Resistor #(.pull(1)) pull_resistor_6 (.node(L_5_9518e519));
  Transistor #(.\type ("n")) transistor_24 (.in(1'b0), .out(L_4_558283f2), .gate(or_1_out));
  Transistor #(.\type ("n")) transistor_25 (.in(1'b0), .out(L_5_9518e519), .gate(or_1_out));
  Transistor #(.\type ("n")) transistor_26 (.in(1'b0), .out(L_4_558283f2), .gate(not_3_out));
  Transistor #(.\type ("n")) transistor_27 (.in(1'b0), .out(L_5_9518e519), .gate(not_3_out));
  Transistor #(.\type ("n")) transistor_28 (.in(1'b0), .out(L_5_9518e519), .gate(IR4));
  Transistor #(.\type ("n")) transistor_29 (.in(1'b0), .out(L_4_558283f2), .gate(not_4_out));
  Transistor #(.\type ("n")) transistor_30 (.in(1'b0), .out(L_4_558283f2), .gate(not_5_out));
  Transistor #(.\type ("n")) transistor_31 (.in(1'b0), .out(L_4_558283f2), .gate(IR2));
  Transistor #(.\type ("n")) transistor_32 (.in(1'b0), .out(L_4_558283f2), .gate(IR6));
  Transistor #(.\type ("n")) transistor_33 (.in(1'b0), .out(L_5_9518e519), .gate(not_7_out));
  Transistor #(.\type ("n")) transistor_34 (.in(1'b0), .out(L_4_558283f2), .gate(IR5));
  Transistor #(.\type ("n")) transistor_35 (.in(1'b0), .out(L_5_9518e519), .gate(IR5));
  Transistor #(.\type ("n")) transistor_36 (.in(1'b0), .out(L_4_558283f2), .gate(L_T0_5a901129));
  Transistor #(.\type ("n")) transistor_37 (.in(1'b0), .out(L_5_9518e519), .gate(L_T0_5a901129));
  Pull_Resistor #(.pull(1)) pull_resistor_7 (.node(L_6_5b7e39b9));
  Transistor #(.\type ("n")) transistor_38 (.in(1'b0), .out(L_6_5b7e39b9), .gate(L_T2_37fe4d42));
  Transistor #(.\type ("n")) transistor_39 (.in(1'b0), .out(L_6_5b7e39b9), .gate(not_4_out));
  Transistor #(.\type ("n")) transistor_40 (.in(1'b0), .out(L_6_5b7e39b9), .gate(not_6_out));
  Pull_Resistor #(.pull(1)) pull_resistor_8 (.node(L_7_14ab2533));
  Transistor #(.\type ("n")) transistor_41 (.in(1'b0), .out(L_7_14ab2533), .gate(not_1_out));
  Transistor #(.\type ("n")) transistor_42 (.in(1'b0), .out(L_7_14ab2533), .gate(not_3_out));
  Transistor #(.\type ("n")) transistor_43 (.in(1'b0), .out(L_7_14ab2533), .gate(IR6));
  Pull_Resistor #(.pull(1)) pull_resistor_9 (.node(L_8_05eb4f56));
  Pull_Resistor #(.pull(1)) pull_resistor_10 (.node(L_9_0082242d));
  Transistor #(.\type ("n")) transistor_44 (.in(1'b0), .out(L_8_05eb4f56), .gate(L_T2_37fe4d42));
  Transistor #(.\type ("n")) transistor_45 (.in(1'b0), .out(L_9_0082242d), .gate(not_1_out));
  Transistor #(.\type ("n")) transistor_46 (.in(1'b0), .out(L_8_05eb4f56), .gate(not_2_out));
  Transistor #(.\type ("n")) transistor_47 (.in(1'b0), .out(L_9_0082242d), .gate(not_3_out));
  Transistor #(.\type ("n")) transistor_48 (.in(1'b0), .out(L_8_05eb4f56), .gate(IR4));
  Transistor #(.\type ("n")) transistor_49 (.in(1'b0), .out(L_9_0082242d), .gate(IR4));
  Transistor #(.\type ("n")) transistor_50 (.in(1'b0), .out(L_8_05eb4f56), .gate(IR3));
  Transistor #(.\type ("n")) transistor_51 (.in(1'b0), .out(L_9_0082242d), .gate(not_5_out));
  Transistor #(.\type ("n")) transistor_52 (.in(1'b0), .out(L_8_05eb4f56), .gate(IR2));
  Transistor #(.\type ("n")) transistor_53 (.in(1'b0), .out(L_9_0082242d), .gate(IR2));
  Transistor #(.\type ("n")) transistor_54 (.in(1'b0), .out(L_9_0082242d), .gate(IR6));
  Transistor #(.\type ("n")) transistor_55 (.in(1'b0), .out(L_9_0082242d), .gate(IR5));
  Transistor #(.\type ("n")) transistor_56 (.in(1'b0), .out(L_9_0082242d), .gate(L_T0_5a901129));
  Pull_Resistor #(.pull(1)) pull_resistor_11 (.node(L_10_57b0d741));
  Transistor #(.\type ("n")) transistor_57 (.in(1'b0), .out(L_10_57b0d741), .gate(not_1_out));
  Transistor #(.\type ("n")) transistor_58 (.in(1'b0), .out(L_10_57b0d741), .gate(not_3_out));
  Transistor #(.\type ("n")) transistor_59 (.in(1'b0), .out(L_10_57b0d741), .gate(IR4));
  Transistor #(.\type ("n")) transistor_60 (.in(1'b0), .out(L_10_57b0d741), .gate(not_5_out));
  Transistor #(.\type ("n")) transistor_61 (.in(1'b0), .out(L_10_57b0d741), .gate(IR2));
  Transistor #(.\type ("n")) transistor_62 (.in(1'b0), .out(L_10_57b0d741), .gate(not_7_out));
  Transistor #(.\type ("n")) transistor_63 (.in(1'b0), .out(L_10_57b0d741), .gate(IR5));
  Transistor #(.\type ("n")) transistor_64 (.in(1'b0), .out(L_10_57b0d741), .gate(L_T0_5a901129));
  Pull_Resistor #(.pull(1)) pull_resistor_12 (.node(L_11_aa2e7fa3));
  Transistor #(.\type ("n")) transistor_65 (.in(1'b0), .out(L_11_aa2e7fa3), .gate(or_1_out));
  Transistor #(.\type ("n")) transistor_66 (.in(1'b0), .out(L_11_aa2e7fa3), .gate(not_3_out));
  Transistor #(.\type ("n")) transistor_67 (.in(1'b0), .out(L_11_aa2e7fa3), .gate(IR4));
  Transistor #(.\type ("n")) transistor_68 (.in(1'b0), .out(L_11_aa2e7fa3), .gate(not_7_out));
  Transistor #(.\type ("n")) transistor_69 (.in(1'b0), .out(L_11_aa2e7fa3), .gate(not_8_out));
  Transistor #(.\type ("n")) transistor_70 (.in(1'b0), .out(L_11_aa2e7fa3), .gate(L_T0_5a901129));
  Pull_Resistor #(.pull(1)) pull_resistor_13 (.node(L_12_85a3418f));
  Pull_Resistor #(.pull(1)) pull_resistor_14 (.node(L_13_587da886));
  Transistor #(.\type ("n")) transistor_71 (.in(1'b0), .out(L_12_85a3418f), .gate(not_1_out));
  Transistor #(.\type ("n")) transistor_72 (.in(1'b0), .out(L_13_587da886), .gate(not_1_out));
  Transistor #(.\type ("n")) transistor_73 (.in(1'b0), .out(L_12_85a3418f), .gate(not_3_out));
  Transistor #(.\type ("n")) transistor_74 (.in(1'b0), .out(L_13_587da886), .gate(not_3_out));
  Transistor #(.\type ("n")) transistor_75 (.in(1'b0), .out(L_13_587da886), .gate(not_4_out));
  Transistor #(.\type ("n")) transistor_76 (.in(1'b0), .out(L_13_587da886), .gate(not_5_out));
  Transistor #(.\type ("n")) transistor_77 (.in(1'b0), .out(L_13_587da886), .gate(IR2));
  Transistor #(.\type ("n")) transistor_78 (.in(1'b0), .out(L_12_85a3418f), .gate(IR6));
  Transistor #(.\type ("n")) transistor_79 (.in(1'b0), .out(L_13_587da886), .gate(IR6));
  Transistor #(.\type ("n")) transistor_80 (.in(1'b0), .out(L_12_85a3418f), .gate(IR5));
  Transistor #(.\type ("n")) transistor_81 (.in(1'b0), .out(L_13_587da886), .gate(IR5));
  Transistor #(.\type ("n")) transistor_82 (.in(1'b0), .out(L_13_587da886), .gate(L_T0_5a901129));
  Pull_Resistor #(.pull(1)) pull_resistor_15 (.node(L_14_4f483598));
  Transistor #(.\type ("n")) transistor_83 (.in(1'b0), .out(L_14_4f483598), .gate(not_1_out));
  Transistor #(.\type ("n")) transistor_84 (.in(1'b0), .out(L_14_4f483598), .gate(not_3_out));
  Transistor #(.\type ("n")) transistor_85 (.in(1'b0), .out(L_14_4f483598), .gate(IR6));
  Transistor #(.\type ("n")) transistor_86 (.in(1'b0), .out(L_14_4f483598), .gate(not_8_out));
  Transistor #(.\type ("n")) transistor_87 (.in(1'b0), .out(L_14_4f483598), .gate(L_T0_5a901129));
  Pull_Resistor #(.pull(1)) pull_resistor_16 (.node(L_15_5dad5732));
  Transistor #(.\type ("n")) transistor_88 (.in(1'b0), .out(L_15_5dad5732), .gate(not_1_out));
  Transistor #(.\type ("n")) transistor_89 (.in(1'b0), .out(L_15_5dad5732), .gate(not_3_out));
  Transistor #(.\type ("n")) transistor_90 (.in(1'b0), .out(L_15_5dad5732), .gate(IR4));
  Transistor #(.\type ("n")) transistor_91 (.in(1'b0), .out(L_15_5dad5732), .gate(not_5_out));
  Transistor #(.\type ("n")) transistor_92 (.in(1'b0), .out(L_15_5dad5732), .gate(IR2));
  Transistor #(.\type ("n")) transistor_93 (.in(1'b0), .out(L_15_5dad5732), .gate(not_7_out));
  Transistor #(.\type ("n")) transistor_94 (.in(1'b0), .out(L_15_5dad5732), .gate(IR5));
  Transistor #(.\type ("n")) transistor_95 (.in(1'b0), .out(L_15_5dad5732), .gate(L_T1X_624de7e6));
  Pull_Resistor #(.pull(1)) pull_resistor_17 (.node(L_16_c7396848));
  Pull_Resistor #(.pull(1)) pull_resistor_18 (.node(L_17_0f5278c7));
  Transistor #(.\type ("n")) transistor_96 (.in(1'b0), .out(L_17_0f5278c7), .gate(not_1_out));
  Transistor #(.\type ("n")) transistor_97 (.in(1'b0), .out(L_16_c7396848), .gate(or_1_out));
  Transistor #(.\type ("n")) transistor_98 (.in(1'b0), .out(L_16_c7396848), .gate(not_3_out));
  Transistor #(.\type ("n")) transistor_99 (.in(1'b0), .out(L_17_0f5278c7), .gate(not_3_out));
  Transistor #(.\type ("n")) transistor_100 (.in(1'b0), .out(L_16_c7396848), .gate(IR4));
  Transistor #(.\type ("n")) transistor_101 (.in(1'b0), .out(L_17_0f5278c7), .gate(not_4_out));
  Transistor #(.\type ("n")) transistor_102 (.in(1'b0), .out(L_16_c7396848), .gate(not_5_out));
  Transistor #(.\type ("n")) transistor_103 (.in(1'b0), .out(L_17_0f5278c7), .gate(not_5_out));
  Transistor #(.\type ("n")) transistor_104 (.in(1'b0), .out(L_16_c7396848), .gate(IR2));
  Transistor #(.\type ("n")) transistor_105 (.in(1'b0), .out(L_17_0f5278c7), .gate(IR2));
  Transistor #(.\type ("n")) transistor_106 (.in(1'b0), .out(L_17_0f5278c7), .gate(IR6));
  Transistor #(.\type ("n")) transistor_107 (.in(1'b0), .out(L_16_c7396848), .gate(not_7_out));
  Transistor #(.\type ("n")) transistor_108 (.in(1'b0), .out(L_16_c7396848), .gate(not_8_out));
  Transistor #(.\type ("n")) transistor_109 (.in(1'b0), .out(L_17_0f5278c7), .gate(not_8_out));
  Transistor #(.\type ("n")) transistor_110 (.in(1'b0), .out(L_17_0f5278c7), .gate(L_T0_5a901129));
  Transistor #(.\type ("n")) transistor_111 (.in(1'b0), .out(L_16_c7396848), .gate(L_T1X_624de7e6));
  Pull_Resistor #(.pull(1)) pull_resistor_19 (.node(L_18_4ab117a9));
  Transistor #(.\type ("n")) transistor_112 (.in(1'b0), .out(L_18_4ab117a9), .gate(or_1_out));
  Transistor #(.\type ("n")) transistor_113 (.in(1'b0), .out(L_18_4ab117a9), .gate(not_3_out));
  Transistor #(.\type ("n")) transistor_114 (.in(1'b0), .out(L_18_4ab117a9), .gate(IR4));
  Transistor #(.\type ("n")) transistor_115 (.in(1'b0), .out(L_18_4ab117a9), .gate(not_5_out));
  Transistor #(.\type ("n")) transistor_116 (.in(1'b0), .out(L_18_4ab117a9), .gate(IR2));
  Transistor #(.\type ("n")) transistor_117 (.in(1'b0), .out(L_18_4ab117a9), .gate(IR5));
  Transistor #(.\type ("n")) transistor_118 (.in(1'b0), .out(L_18_4ab117a9), .gate(L_T1X_624de7e6));
  Pull_Resistor #(.pull(1)) pull_resistor_20 (.node(L_19_e094c090));
  Transistor #(.\type ("n")) transistor_119 (.in(1'b0), .out(L_19_e094c090), .gate(or_1_out));
  Transistor #(.\type ("n")) transistor_120 (.in(1'b0), .out(L_19_e094c090), .gate(not_3_out));
  Transistor #(.\type ("n")) transistor_121 (.in(1'b0), .out(L_19_e094c090), .gate(not_6_out));
  Transistor #(.\type ("n")) transistor_122 (.in(1'b0), .out(L_19_e094c090), .gate(IR6));
  Transistor #(.\type ("n")) transistor_123 (.in(1'b0), .out(L_19_e094c090), .gate(not_8_out));
  Transistor #(.\type ("n")) transistor_124 (.in(1'b0), .out(L_19_e094c090), .gate(L_T0_5a901129));
  Pull_Resistor #(.pull(1)) pull_resistor_21 (.node(L_20_adeacd1b));
  Transistor #(.\type ("n")) transistor_125 (.in(1'b0), .out(L_20_adeacd1b), .gate(or_1_out));
  Transistor #(.\type ("n")) transistor_126 (.in(1'b0), .out(L_20_adeacd1b), .gate(not_3_out));
  Transistor #(.\type ("n")) transistor_127 (.in(1'b0), .out(L_20_adeacd1b), .gate(IR4));
  Transistor #(.\type ("n")) transistor_128 (.in(1'b0), .out(L_20_adeacd1b), .gate(IR6));
  Transistor #(.\type ("n")) transistor_129 (.in(1'b0), .out(L_20_adeacd1b), .gate(not_8_out));
  Transistor #(.\type ("n")) transistor_130 (.in(1'b0), .out(L_20_adeacd1b), .gate(L_T0_5a901129));
  Pull_Resistor #(.pull(1)) pull_resistor_22 (.node(L_21_ada5c31c));
  Transistor #(.\type ("n")) transistor_131 (.in(1'b0), .out(L_21_ada5c31c), .gate(or_1_out));
  Transistor #(.\type ("n")) transistor_132 (.in(1'b0), .out(L_21_ada5c31c), .gate(IR7));
  Transistor #(.\type ("n")) transistor_133 (.in(1'b0), .out(L_21_ada5c31c), .gate(IR4));
  Transistor #(.\type ("n")) transistor_134 (.in(1'b0), .out(L_21_ada5c31c), .gate(IR3));
  Transistor #(.\type ("n")) transistor_135 (.in(1'b0), .out(L_21_ada5c31c), .gate(IR2));
  Transistor #(.\type ("n")) transistor_136 (.in(1'b0), .out(L_21_ada5c31c), .gate(IR6));
  Transistor #(.\type ("n")) transistor_137 (.in(1'b0), .out(L_21_ada5c31c), .gate(not_8_out));
  Transistor #(.\type ("n")) transistor_138 (.in(1'b0), .out(L_21_ada5c31c), .gate(L_T0_5a901129));
  Pull_Resistor #(.pull(1)) pull_resistor_23 (.node(L_22_f545d19e));
  Transistor #(.\type ("n")) transistor_139 (.in(1'b0), .out(L_22_f545d19e), .gate(L_T5_89b31bc6));
  Transistor #(.\type ("n")) transistor_140 (.in(1'b0), .out(L_22_f545d19e), .gate(or_1_out));
  Transistor #(.\type ("n")) transistor_141 (.in(1'b0), .out(L_22_f545d19e), .gate(IR7));
  Transistor #(.\type ("n")) transistor_142 (.in(1'b0), .out(L_22_f545d19e), .gate(IR4));
  Transistor #(.\type ("n")) transistor_143 (.in(1'b0), .out(L_22_f545d19e), .gate(IR3));
  Transistor #(.\type ("n")) transistor_144 (.in(1'b0), .out(L_22_f545d19e), .gate(IR2));
  Transistor #(.\type ("n")) transistor_145 (.in(1'b0), .out(L_22_f545d19e), .gate(IR6));
  Transistor #(.\type ("n")) transistor_146 (.in(1'b0), .out(L_22_f545d19e), .gate(IR5));
  Pull_Resistor #(.pull(1)) pull_resistor_24 (.node(L_23_d0835dd9));
  Transistor #(.\type ("n")) transistor_147 (.in(1'b0), .out(L_23_d0835dd9), .gate(or_1_out));
  Transistor #(.\type ("n")) transistor_148 (.in(1'b0), .out(L_23_d0835dd9), .gate(IR7));
  Transistor #(.\type ("n")) transistor_149 (.in(1'b0), .out(L_23_d0835dd9), .gate(IR4));
  Transistor #(.\type ("n")) transistor_150 (.in(1'b0), .out(L_23_d0835dd9), .gate(not_5_out));
  Transistor #(.\type ("n")) transistor_151 (.in(1'b0), .out(L_23_d0835dd9), .gate(IR2));
  Transistor #(.\type ("n")) transistor_152 (.in(1'b0), .out(L_23_d0835dd9), .gate(IR5));
  Transistor #(.\type ("n")) transistor_153 (.in(1'b0), .out(L_23_d0835dd9), .gate(L_T0_5a901129));
  Pull_Resistor #(.pull(1)) pull_resistor_25 (.node(L_24_b6efc2f4));
  Pull_Resistor #(.pull(1)) pull_resistor_26 (.node(L_25_f5ad6aee));
  Transistor #(.\type ("n")) transistor_154 (.in(1'b0), .out(L_24_b6efc2f4), .gate(L_T4_d9b6e407));
  Transistor #(.\type ("n")) transistor_155 (.in(1'b0), .out(L_25_f5ad6aee), .gate(L_T3_3fe619b3));
  Transistor #(.\type ("n")) transistor_156 (.in(1'b0), .out(L_24_b6efc2f4), .gate(or_1_out));
  Transistor #(.\type ("n")) transistor_157 (.in(1'b0), .out(L_25_f5ad6aee), .gate(or_1_out));
  Transistor #(.\type ("n")) transistor_158 (.in(1'b0), .out(L_24_b6efc2f4), .gate(IR7));
  Transistor #(.\type ("n")) transistor_159 (.in(1'b0), .out(L_25_f5ad6aee), .gate(IR7));
  Transistor #(.\type ("n")) transistor_160 (.in(1'b0), .out(L_24_b6efc2f4), .gate(IR4));
  Transistor #(.\type ("n")) transistor_161 (.in(1'b0), .out(L_25_f5ad6aee), .gate(IR4));
  Transistor #(.\type ("n")) transistor_162 (.in(1'b0), .out(L_24_b6efc2f4), .gate(IR3));
  Transistor #(.\type ("n")) transistor_163 (.in(1'b0), .out(L_25_f5ad6aee), .gate(not_5_out));
  Transistor #(.\type ("n")) transistor_164 (.in(1'b0), .out(L_24_b6efc2f4), .gate(IR2));
  Transistor #(.\type ("n")) transistor_165 (.in(1'b0), .out(L_25_f5ad6aee), .gate(IR2));
  Transistor #(.\type ("n")) transistor_166 (.in(1'b0), .out(L_24_b6efc2f4), .gate(not_7_out));
  Transistor #(.\type ("n")) transistor_167 (.in(1'b0), .out(L_24_b6efc2f4), .gate(not_8_out));
  Transistor #(.\type ("n")) transistor_168 (.in(1'b0), .out(L_25_f5ad6aee), .gate(not_8_out));
  Pull_Resistor #(.pull(1)) pull_resistor_27 (.node(L_26_ffeee2da));
  Transistor #(.\type ("n")) transistor_169 (.in(1'b0), .out(L_26_ffeee2da), .gate(L_T5_89b31bc6));
  Transistor #(.\type ("n")) transistor_170 (.in(1'b0), .out(L_26_ffeee2da), .gate(or_1_out));
  Transistor #(.\type ("n")) transistor_171 (.in(1'b0), .out(L_26_ffeee2da), .gate(IR7));
  Transistor #(.\type ("n")) transistor_172 (.in(1'b0), .out(L_26_ffeee2da), .gate(IR4));
  Transistor #(.\type ("n")) transistor_173 (.in(1'b0), .out(L_26_ffeee2da), .gate(IR3));
  Transistor #(.\type ("n")) transistor_174 (.in(1'b0), .out(L_26_ffeee2da), .gate(IR2));
  Transistor #(.\type ("n")) transistor_175 (.in(1'b0), .out(L_26_ffeee2da), .gate(not_7_out));
  Transistor #(.\type ("n")) transistor_176 (.in(1'b0), .out(L_26_ffeee2da), .gate(IR5));
  Pull_Resistor #(.pull(1)) pull_resistor_28 (.node(L_27_6492a6f4));
  Transistor #(.\type ("n")) transistor_177 (.in(1'b0), .out(L_27_6492a6f4), .gate(not_1_out));
  Transistor #(.\type ("n")) transistor_178 (.in(1'b0), .out(L_27_6492a6f4), .gate(IR7));
  Transistor #(.\type ("n")) transistor_179 (.in(1'b0), .out(L_27_6492a6f4), .gate(not_7_out));
  Transistor #(.\type ("n")) transistor_180 (.in(1'b0), .out(L_27_6492a6f4), .gate(not_8_out));
  Pull_Resistor #(.pull(1)) pull_resistor_29 (.node(L_28_647e552a));
  Pull_Resistor #(.pull(1)) pull_resistor_30 (.node(L_29_1d3a3eb3));
  Transistor #(.\type ("n")) transistor_181 (.in(1'b0), .out(L_28_647e552a), .gate(L_T2_37fe4d42));
  Transistor #(.\type ("n")) transistor_182 (.in(1'b0), .out(L_29_1d3a3eb3), .gate(not_2_out));
  Transistor #(.\type ("n")) transistor_183 (.in(1'b0), .out(L_29_1d3a3eb3), .gate(IR7));
  Transistor #(.\type ("n")) transistor_184 (.in(1'b0), .out(L_29_1d3a3eb3), .gate(not_7_out));
  Transistor #(.\type ("n")) transistor_185 (.in(1'b0), .out(L_29_1d3a3eb3), .gate(IR5));
  Transistor #(.\type ("n")) transistor_186 (.in(1'b0), .out(L_29_1d3a3eb3), .gate(L_T0_5a901129));
  Pull_Resistor #(.pull(1)) pull_resistor_31 (.node(L_30_3bf8f3d0));
  Transistor #(.\type ("n")) transistor_187 (.in(1'b0), .out(L_30_3bf8f3d0), .gate(or_1_out));
  Transistor #(.\type ("n")) transistor_188 (.in(1'b0), .out(L_30_3bf8f3d0), .gate(IR7));
  Transistor #(.\type ("n")) transistor_189 (.in(1'b0), .out(L_30_3bf8f3d0), .gate(IR4));
  Transistor #(.\type ("n")) transistor_190 (.in(1'b0), .out(L_30_3bf8f3d0), .gate(not_5_out));
  Transistor #(.\type ("n")) transistor_191 (.in(1'b0), .out(L_30_3bf8f3d0), .gate(not_6_out));
  Transistor #(.\type ("n")) transistor_192 (.in(1'b0), .out(L_30_3bf8f3d0), .gate(not_7_out));
  Pull_Resistor #(.pull(1)) pull_resistor_32 (.node(L_31_e958c8e2));
  Transistor #(.\type ("n")) transistor_193 (.in(1'b0), .out(L_31_e958c8e2), .gate(L_T2_37fe4d42));
  Transistor #(.\type ("n")) transistor_194 (.in(1'b0), .out(L_31_e958c8e2), .gate(IR4));
  Transistor #(.\type ("n")) transistor_195 (.in(1'b0), .out(L_31_e958c8e2), .gate(not_5_out));
  Transistor #(.\type ("n")) transistor_196 (.in(1'b0), .out(L_31_e958c8e2), .gate(not_6_out));
  Pull_Resistor #(.pull(1)) pull_resistor_33 (.node(L_32_7de83e69));
  Pull_Resistor #(.pull(1)) pull_resistor_34 (.node(L_33_cae225fb));
  Transistor #(.\type ("n")) transistor_197 (.in(1'b0), .out(L_33_cae225fb), .gate(L_T2_37fe4d42));
  Transistor #(.\type ("n")) transistor_198 (.in(1'b0), .out(L_32_7de83e69), .gate(not_2_out));
  Transistor #(.\type ("n")) transistor_199 (.in(1'b0), .out(L_32_7de83e69), .gate(IR7));
  Transistor #(.\type ("n")) transistor_200 (.in(1'b0), .out(L_33_cae225fb), .gate(IR3));
  Transistor #(.\type ("n")) transistor_201 (.in(1'b0), .out(L_32_7de83e69), .gate(IR6));
  Transistor #(.\type ("n")) transistor_202 (.in(1'b0), .out(L_32_7de83e69), .gate(IR5));
  Transistor #(.\type ("n")) transistor_203 (.in(1'b0), .out(L_32_7de83e69), .gate(L_T0_5a901129));
  Pull_Resistor #(.pull(1)) pull_resistor_35 (.node(L_34_97db28cb));
  Transistor #(.\type ("n")) transistor_204 (.in(1'b0), .out(L_34_97db28cb), .gate(L_T0_5a901129));
  Pull_Resistor #(.pull(1)) pull_resistor_36 (.node(L_35_8b2262aa));
  Transistor #(.\type ("n")) transistor_205 (.in(1'b0), .out(L_35_8b2262aa), .gate(L_T2_37fe4d42));
  Transistor #(.\type ("n")) transistor_206 (.in(1'b0), .out(L_35_8b2262aa), .gate(or_1_out));
  Transistor #(.\type ("n")) transistor_207 (.in(1'b0), .out(L_35_8b2262aa), .gate(IR7));
  Transistor #(.\type ("n")) transistor_208 (.in(1'b0), .out(L_35_8b2262aa), .gate(IR4));
  Transistor #(.\type ("n")) transistor_209 (.in(1'b0), .out(L_35_8b2262aa), .gate(IR2));
  Pull_Resistor #(.pull(1)) pull_resistor_37 (.node(L_36_34609549));
  Transistor #(.\type ("n")) transistor_210 (.in(1'b0), .out(L_36_34609549), .gate(L_T3_3fe619b3));
  Transistor #(.\type ("n")) transistor_211 (.in(1'b0), .out(L_36_34609549), .gate(or_1_out));
  Transistor #(.\type ("n")) transistor_212 (.in(1'b0), .out(L_36_34609549), .gate(IR7));
  Transistor #(.\type ("n")) transistor_213 (.in(1'b0), .out(L_36_34609549), .gate(IR4));
  Pull_Resistor #(.pull(1)) pull_resistor_38 (.node(L_37_acfb42d2));
  Transistor #(.\type ("n")) transistor_214 (.in(1'b0), .out(L_37_acfb42d2), .gate(L_T4_d9b6e407));
  Transistor #(.\type ("n")) transistor_215 (.in(1'b0), .out(L_37_acfb42d2), .gate(or_1_out));
  Transistor #(.\type ("n")) transistor_216 (.in(1'b0), .out(L_37_acfb42d2), .gate(IR7));
  Transistor #(.\type ("n")) transistor_217 (.in(1'b0), .out(L_37_acfb42d2), .gate(IR4));
  Transistor #(.\type ("n")) transistor_218 (.in(1'b0), .out(L_37_acfb42d2), .gate(IR3));
  Transistor #(.\type ("n")) transistor_219 (.in(1'b0), .out(L_37_acfb42d2), .gate(IR2));
  Transistor #(.\type ("n")) transistor_220 (.in(1'b0), .out(L_37_acfb42d2), .gate(IR6));
  Pull_Resistor #(.pull(1)) pull_resistor_39 (.node(L_38_43aa51c3));
  Transistor #(.\type ("n")) transistor_221 (.in(1'b0), .out(L_38_43aa51c3), .gate(L_T4_d9b6e407));
  Transistor #(.\type ("n")) transistor_222 (.in(1'b0), .out(L_38_43aa51c3), .gate(or_1_out));
  Transistor #(.\type ("n")) transistor_223 (.in(1'b0), .out(L_38_43aa51c3), .gate(IR7));
  Transistor #(.\type ("n")) transistor_224 (.in(1'b0), .out(L_38_43aa51c3), .gate(IR4));
  Transistor #(.\type ("n")) transistor_225 (.in(1'b0), .out(L_38_43aa51c3), .gate(IR3));
  Transistor #(.\type ("n")) transistor_226 (.in(1'b0), .out(L_38_43aa51c3), .gate(IR2));
  Transistor #(.\type ("n")) transistor_227 (.in(1'b0), .out(L_38_43aa51c3), .gate(not_7_out));
  Transistor #(.\type ("n")) transistor_228 (.in(1'b0), .out(L_38_43aa51c3), .gate(IR5));
  Pull_Resistor #(.pull(1)) pull_resistor_40 (.node(L_39_c97a3f22));
  Pull_Resistor #(.pull(1)) pull_resistor_41 (.node(L_40_1e6b68e0));
  Transistor #(.\type ("n")) transistor_229 (.in(1'b0), .out(L_40_1e6b68e0), .gate(L_T4_d9b6e407));
  Transistor #(.\type ("n")) transistor_230 (.in(1'b0), .out(L_39_c97a3f22), .gate(L_T3_3fe619b3));
  Transistor #(.\type ("n")) transistor_231 (.in(1'b0), .out(L_39_c97a3f22), .gate(not_2_out));
  Transistor #(.\type ("n")) transistor_232 (.in(1'b0), .out(L_40_1e6b68e0), .gate(not_2_out));
  Transistor #(.\type ("n")) transistor_233 (.in(1'b0), .out(L_39_c97a3f22), .gate(IR4));
  Transistor #(.\type ("n")) transistor_234 (.in(1'b0), .out(L_40_1e6b68e0), .gate(not_4_out));
  Transistor #(.\type ("n")) transistor_235 (.in(1'b0), .out(L_39_c97a3f22), .gate(IR3));
  Transistor #(.\type ("n")) transistor_236 (.in(1'b0), .out(L_40_1e6b68e0), .gate(IR3));
  Transistor #(.\type ("n")) transistor_237 (.in(1'b0), .out(L_39_c97a3f22), .gate(IR2));
  Transistor #(.\type ("n")) transistor_238 (.in(1'b0), .out(L_40_1e6b68e0), .gate(IR2));
  Pull_Resistor #(.pull(1)) pull_resistor_42 (.node(L_41_b24af141));
  Transistor #(.\type ("n")) transistor_239 (.in(1'b0), .out(L_41_b24af141), .gate(L_T2_37fe4d42));
  Transistor #(.\type ("n")) transistor_240 (.in(1'b0), .out(L_41_b24af141), .gate(not_2_out));
  Transistor #(.\type ("n")) transistor_241 (.in(1'b0), .out(L_41_b24af141), .gate(not_4_out));
  Transistor #(.\type ("n")) transistor_242 (.in(1'b0), .out(L_41_b24af141), .gate(IR3));
  Transistor #(.\type ("n")) transistor_243 (.in(1'b0), .out(L_41_b24af141), .gate(IR2));
  Pull_Resistor #(.pull(1)) pull_resistor_43 (.node(L_42_ae8bf3e0));
  Transistor #(.\type ("n")) transistor_244 (.in(1'b0), .out(L_42_ae8bf3e0), .gate(L_T3_3fe619b3));
  Transistor #(.\type ("n")) transistor_245 (.in(1'b0), .out(L_42_ae8bf3e0), .gate(not_4_out));
  Transistor #(.\type ("n")) transistor_246 (.in(1'b0), .out(L_42_ae8bf3e0), .gate(not_5_out));
  Pull_Resistor #(.pull(1)) pull_resistor_44 (.node(L_43_fdaf143b));
  Pull_Resistor #(.pull(1)) pull_resistor_45 (.node(L_44_bb416d4b));
  Transistor #(.\type ("n")) transistor_247 (.in(1'b0), .out(L_44_bb416d4b), .gate(not_1_out));
  Transistor #(.\type ("n")) transistor_248 (.in(1'b0), .out(L_43_fdaf143b), .gate(or_1_out));
  Transistor #(.\type ("n")) transistor_249 (.in(1'b0), .out(L_43_fdaf143b), .gate(IR7));
  Transistor #(.\type ("n")) transistor_250 (.in(1'b0), .out(L_44_bb416d4b), .gate(not_3_out));
  Transistor #(.\type ("n")) transistor_251 (.in(1'b0), .out(L_43_fdaf143b), .gate(IR4));
  Transistor #(.\type ("n")) transistor_252 (.in(1'b0), .out(L_43_fdaf143b), .gate(not_5_out));
  Transistor #(.\type ("n")) transistor_253 (.in(1'b0), .out(L_43_fdaf143b), .gate(IR2));
  Transistor #(.\type ("n")) transistor_254 (.in(1'b0), .out(L_44_bb416d4b), .gate(not_7_out));
  Transistor #(.\type ("n")) transistor_255 (.in(1'b0), .out(L_43_fdaf143b), .gate(not_8_out));
  Transistor #(.\type ("n")) transistor_256 (.in(1'b0), .out(L_44_bb416d4b), .gate(not_8_out));
  Pull_Resistor #(.pull(1)) pull_resistor_46 (.node(L_45_e516ed8c));
  Transistor #(.\type ("n")) transistor_257 (.in(1'b0), .out(L_45_e516ed8c), .gate(L_T4_d9b6e407));
  Transistor #(.\type ("n")) transistor_258 (.in(1'b0), .out(L_45_e516ed8c), .gate(not_2_out));
  Transistor #(.\type ("n")) transistor_259 (.in(1'b0), .out(L_45_e516ed8c), .gate(IR4));
  Transistor #(.\type ("n")) transistor_260 (.in(1'b0), .out(L_45_e516ed8c), .gate(IR3));
  Transistor #(.\type ("n")) transistor_261 (.in(1'b0), .out(L_45_e516ed8c), .gate(IR2));
  Pull_Resistor #(.pull(1)) pull_resistor_47 (.node(L_46_6c10990a));
  Transistor #(.\type ("n")) transistor_262 (.in(1'b0), .out(L_46_6c10990a), .gate(L_T3_3fe619b3));
  Transistor #(.\type ("n")) transistor_263 (.in(1'b0), .out(L_46_6c10990a), .gate(not_2_out));
  Transistor #(.\type ("n")) transistor_264 (.in(1'b0), .out(L_46_6c10990a), .gate(not_4_out));
  Transistor #(.\type ("n")) transistor_265 (.in(1'b0), .out(L_46_6c10990a), .gate(IR3));
  Transistor #(.\type ("n")) transistor_266 (.in(1'b0), .out(L_46_6c10990a), .gate(IR2));
  Pull_Resistor #(.pull(1)) pull_resistor_48 (.node(L_47_7c60183d));
  Pull_Resistor #(.pull(1)) pull_resistor_49 (.node(L_48_330a6f3f));
  Transistor #(.\type ("n")) transistor_267 (.in(1'b0), .out(L_48_330a6f3f), .gate(L_T2_37fe4d42));
  Transistor #(.\type ("n")) transistor_268 (.in(1'b0), .out(L_47_7c60183d), .gate(or_1_out));
  Transistor #(.\type ("n")) transistor_269 (.in(1'b0), .out(L_48_330a6f3f), .gate(or_1_out));
  Transistor #(.\type ("n")) transistor_270 (.in(1'b0), .out(L_47_7c60183d), .gate(IR7));
  Transistor #(.\type ("n")) transistor_271 (.in(1'b0), .out(L_48_330a6f3f), .gate(IR7));
  Transistor #(.\type ("n")) transistor_272 (.in(1'b0), .out(L_47_7c60183d), .gate(IR4));
  Transistor #(.\type ("n")) transistor_273 (.in(1'b0), .out(L_48_330a6f3f), .gate(IR4));
  Transistor #(.\type ("n")) transistor_274 (.in(1'b0), .out(L_47_7c60183d), .gate(IR3));
  Transistor #(.\type ("n")) transistor_275 (.in(1'b0), .out(L_48_330a6f3f), .gate(IR3));
  Transistor #(.\type ("n")) transistor_276 (.in(1'b0), .out(L_47_7c60183d), .gate(IR2));
  Transistor #(.\type ("n")) transistor_277 (.in(1'b0), .out(L_48_330a6f3f), .gate(IR2));
  Transistor #(.\type ("n")) transistor_278 (.in(1'b0), .out(L_48_330a6f3f), .gate(IR6));
  Transistor #(.\type ("n")) transistor_279 (.in(1'b0), .out(L_47_7c60183d), .gate(not_7_out));
  Transistor #(.\type ("n")) transistor_280 (.in(1'b0), .out(L_48_330a6f3f), .gate(not_8_out));
  Pull_Resistor #(.pull(1)) pull_resistor_50 (.node(L_49_f70f8148));
  Transistor #(.\type ("n")) transistor_281 (.in(1'b0), .out(L_49_f70f8148), .gate(or_1_out));
  Transistor #(.\type ("n")) transistor_282 (.in(1'b0), .out(L_49_f70f8148), .gate(not_3_out));
  Transistor #(.\type ("n")) transistor_283 (.in(1'b0), .out(L_49_f70f8148), .gate(IR4));
  Transistor #(.\type ("n")) transistor_284 (.in(1'b0), .out(L_49_f70f8148), .gate(not_7_out));
  Transistor #(.\type ("n")) transistor_285 (.in(1'b0), .out(L_49_f70f8148), .gate(L_T0_5a901129));
  Pull_Resistor #(.pull(1)) pull_resistor_51 (.node(L_50_6b408103));
  Transistor #(.\type ("n")) transistor_286 (.in(1'b0), .out(L_50_6b408103), .gate(not_2_out));
  Transistor #(.\type ("n")) transistor_287 (.in(1'b0), .out(L_50_6b408103), .gate(not_3_out));
  Transistor #(.\type ("n")) transistor_288 (.in(1'b0), .out(L_50_6b408103), .gate(not_7_out));
  Transistor #(.\type ("n")) transistor_289 (.in(1'b0), .out(L_50_6b408103), .gate(IR5));
  Transistor #(.\type ("n")) transistor_290 (.in(1'b0), .out(L_50_6b408103), .gate(L_T0_5a901129));
  Pull_Resistor #(.pull(1)) pull_resistor_52 (.node(L_51_79fb832a));
  Pull_Resistor #(.pull(1)) pull_resistor_53 (.node(L_52_253f2da2));
  Transistor #(.\type ("n")) transistor_291 (.in(1'b0), .out(L_51_79fb832a), .gate(not_2_out));
  Transistor #(.\type ("n")) transistor_292 (.in(1'b0), .out(L_52_253f2da2), .gate(not_2_out));
  Transistor #(.\type ("n")) transistor_293 (.in(1'b0), .out(L_51_79fb832a), .gate(not_3_out));
  Transistor #(.\type ("n")) transistor_294 (.in(1'b0), .out(L_51_79fb832a), .gate(not_7_out));
  Transistor #(.\type ("n")) transistor_295 (.in(1'b0), .out(L_52_253f2da2), .gate(not_7_out));
  Transistor #(.\type ("n")) transistor_296 (.in(1'b0), .out(L_51_79fb832a), .gate(not_8_out));
  Transistor #(.\type ("n")) transistor_297 (.in(1'b0), .out(L_52_253f2da2), .gate(not_8_out));
  Transistor #(.\type ("n")) transistor_298 (.in(1'b0), .out(L_51_79fb832a), .gate(L_T0_5a901129));
  Transistor #(.\type ("n")) transistor_299 (.in(1'b0), .out(L_52_253f2da2), .gate(L_T0_5a901129));
  Pull_Resistor #(.pull(1)) pull_resistor_54 (.node(L_53_d08b6e35));
  Transistor #(.\type ("n")) transistor_300 (.in(1'b0), .out(L_53_d08b6e35), .gate(not_1_out));
  Transistor #(.\type ("n")) transistor_301 (.in(1'b0), .out(L_53_d08b6e35), .gate(IR7));
  Transistor #(.\type ("n")) transistor_302 (.in(1'b0), .out(L_53_d08b6e35), .gate(IR6));
  Transistor #(.\type ("n")) transistor_303 (.in(1'b0), .out(L_53_d08b6e35), .gate(not_8_out));
  Pull_Resistor #(.pull(1)) pull_resistor_55 (.node(L_54_01afe50f));
  Transistor #(.\type ("n")) transistor_304 (.in(1'b0), .out(L_54_01afe50f), .gate(L_T3_3fe619b3));
  Transistor #(.\type ("n")) transistor_305 (.in(1'b0), .out(L_54_01afe50f), .gate(or_1_out));
  Transistor #(.\type ("n")) transistor_306 (.in(1'b0), .out(L_54_01afe50f), .gate(IR7));
  Transistor #(.\type ("n")) transistor_307 (.in(1'b0), .out(L_54_01afe50f), .gate(IR4));
  Transistor #(.\type ("n")) transistor_308 (.in(1'b0), .out(L_54_01afe50f), .gate(not_5_out));
  Transistor #(.\type ("n")) transistor_309 (.in(1'b0), .out(L_54_01afe50f), .gate(not_6_out));
  Transistor #(.\type ("n")) transistor_310 (.in(1'b0), .out(L_54_01afe50f), .gate(not_7_out));
  Pull_Resistor #(.pull(1)) pull_resistor_56 (.node(L_55_73ecc214));
  Pull_Resistor #(.pull(1)) pull_resistor_57 (.node(L_56_35bf93dd));
  Transistor #(.\type ("n")) transistor_311 (.in(1'b0), .out(L_56_35bf93dd), .gate(L_T5_89b31bc6));
  Transistor #(.\type ("n")) transistor_312 (.in(1'b0), .out(L_55_73ecc214), .gate(not_1_out));
  Transistor #(.\type ("n")) transistor_313 (.in(1'b0), .out(L_56_35bf93dd), .gate(or_1_out));
  Transistor #(.\type ("n")) transistor_314 (.in(1'b0), .out(L_55_73ecc214), .gate(IR7));
  Transistor #(.\type ("n")) transistor_315 (.in(1'b0), .out(L_56_35bf93dd), .gate(IR7));
  Transistor #(.\type ("n")) transistor_316 (.in(1'b0), .out(L_56_35bf93dd), .gate(IR4));
  Transistor #(.\type ("n")) transistor_317 (.in(1'b0), .out(L_56_35bf93dd), .gate(IR3));
  Transistor #(.\type ("n")) transistor_318 (.in(1'b0), .out(L_56_35bf93dd), .gate(IR2));
  Transistor #(.\type ("n")) transistor_319 (.in(1'b0), .out(L_55_73ecc214), .gate(IR6));
  Transistor #(.\type ("n")) transistor_320 (.in(1'b0), .out(L_56_35bf93dd), .gate(IR6));
  Transistor #(.\type ("n")) transistor_321 (.in(1'b0), .out(L_56_35bf93dd), .gate(not_8_out));
  Pull_Resistor #(.pull(1)) pull_resistor_58 (.node(L_57_0f0af090));
  Transistor #(.\type ("n")) transistor_322 (.in(1'b0), .out(L_57_0f0af090), .gate(L_T2_37fe4d42));
  Transistor #(.\type ("n")) transistor_323 (.in(1'b0), .out(L_57_0f0af090), .gate(or_1_out));
  Transistor #(.\type ("n")) transistor_324 (.in(1'b0), .out(L_57_0f0af090), .gate(IR7));
  Transistor #(.\type ("n")) transistor_325 (.in(1'b0), .out(L_57_0f0af090), .gate(IR4));
  Transistor #(.\type ("n")) transistor_326 (.in(1'b0), .out(L_57_0f0af090), .gate(IR2));
  Pull_Resistor #(.pull(1)) pull_resistor_59 (.node(L_58_4e7562c2));
  Transistor #(.\type ("n")) transistor_327 (.in(1'b0), .out(L_58_4e7562c2), .gate(or_1_out));
  Transistor #(.\type ("n")) transistor_328 (.in(1'b0), .out(L_58_4e7562c2), .gate(not_3_out));
  Transistor #(.\type ("n")) transistor_329 (.in(1'b0), .out(L_58_4e7562c2), .gate(not_4_out));
  Transistor #(.\type ("n")) transistor_330 (.in(1'b0), .out(L_58_4e7562c2), .gate(not_5_out));
  Transistor #(.\type ("n")) transistor_331 (.in(1'b0), .out(L_58_4e7562c2), .gate(IR2));
  Transistor #(.\type ("n")) transistor_332 (.in(1'b0), .out(L_58_4e7562c2), .gate(IR6));
  Transistor #(.\type ("n")) transistor_333 (.in(1'b0), .out(L_58_4e7562c2), .gate(IR5));
  Transistor #(.\type ("n")) transistor_334 (.in(1'b0), .out(L_58_4e7562c2), .gate(L_T0_5a901129));
  Pull_Resistor #(.pull(1)) pull_resistor_60 (.node(L_59_d4e3d539));
  Pull_Resistor #(.pull(1)) pull_resistor_61 (.node(L_60_8c46ae22));
  Transistor #(.\type ("n")) transistor_335 (.in(1'b0), .out(L_59_d4e3d539), .gate(not_2_out));
  Transistor #(.\type ("n")) transistor_336 (.in(1'b0), .out(L_60_8c46ae22), .gate(not_2_out));
  Transistor #(.\type ("n")) transistor_337 (.in(1'b0), .out(L_59_d4e3d539), .gate(IR7));
  Transistor #(.\type ("n")) transistor_338 (.in(1'b0), .out(L_60_8c46ae22), .gate(not_7_out));
  Transistor #(.\type ("n")) transistor_339 (.in(1'b0), .out(L_60_8c46ae22), .gate(not_8_out));
  Transistor #(.\type ("n")) transistor_340 (.in(1'b0), .out(L_59_d4e3d539), .gate(L_T1X_624de7e6));
  Transistor #(.\type ("n")) transistor_341 (.in(1'b0), .out(L_60_8c46ae22), .gate(L_T1X_624de7e6));
  Pull_Resistor #(.pull(1)) pull_resistor_62 (.node(L_61_ef440803));
  Transistor #(.\type ("n")) transistor_342 (.in(1'b0), .out(L_61_ef440803), .gate(not_1_out));
  Transistor #(.\type ("n")) transistor_343 (.in(1'b0), .out(L_61_ef440803), .gate(IR7));
  Transistor #(.\type ("n")) transistor_344 (.in(1'b0), .out(L_61_ef440803), .gate(IR4));
  Transistor #(.\type ("n")) transistor_345 (.in(1'b0), .out(L_61_ef440803), .gate(IR2));
  Transistor #(.\type ("n")) transistor_346 (.in(1'b0), .out(L_61_ef440803), .gate(L_T1X_624de7e6));
  Pull_Resistor #(.pull(1)) pull_resistor_63 (.node(L_62_1470bf03));
  Transistor #(.\type ("n")) transistor_347 (.in(1'b0), .out(L_62_1470bf03), .gate(not_1_out));
  Transistor #(.\type ("n")) transistor_348 (.in(1'b0), .out(L_62_1470bf03), .gate(not_3_out));
  Transistor #(.\type ("n")) transistor_349 (.in(1'b0), .out(L_62_1470bf03), .gate(IR4));
  Transistor #(.\type ("n")) transistor_350 (.in(1'b0), .out(L_62_1470bf03), .gate(not_5_out));
  Transistor #(.\type ("n")) transistor_351 (.in(1'b0), .out(L_62_1470bf03), .gate(IR2));
  Transistor #(.\type ("n")) transistor_352 (.in(1'b0), .out(L_62_1470bf03), .gate(IR6));
  Transistor #(.\type ("n")) transistor_353 (.in(1'b0), .out(L_62_1470bf03), .gate(IR5));
  Transistor #(.\type ("n")) transistor_354 (.in(1'b0), .out(L_62_1470bf03), .gate(L_T0_5a901129));
  Pull_Resistor #(.pull(1)) pull_resistor_64 (.node(L_63_0a5e7e38));
  Pull_Resistor #(.pull(1)) pull_resistor_65 (.node(L_64_e6cb4ce5));
  Transistor #(.\type ("n")) transistor_355 (.in(1'b0), .out(L_63_0a5e7e38), .gate(or_1_out));
  Transistor #(.\type ("n")) transistor_356 (.in(1'b0), .out(L_64_e6cb4ce5), .gate(not_2_out));
  Transistor #(.\type ("n")) transistor_357 (.in(1'b0), .out(L_63_0a5e7e38), .gate(IR7));
  Transistor #(.\type ("n")) transistor_358 (.in(1'b0), .out(L_64_e6cb4ce5), .gate(not_3_out));
  Transistor #(.\type ("n")) transistor_359 (.in(1'b0), .out(L_63_0a5e7e38), .gate(IR4));
  Transistor #(.\type ("n")) transistor_360 (.in(1'b0), .out(L_63_0a5e7e38), .gate(not_5_out));
  Transistor #(.\type ("n")) transistor_361 (.in(1'b0), .out(L_63_0a5e7e38), .gate(IR2));
  Transistor #(.\type ("n")) transistor_362 (.in(1'b0), .out(L_64_e6cb4ce5), .gate(IR6));
  Transistor #(.\type ("n")) transistor_363 (.in(1'b0), .out(L_63_0a5e7e38), .gate(not_7_out));
  Transistor #(.\type ("n")) transistor_364 (.in(1'b0), .out(L_63_0a5e7e38), .gate(not_8_out));
  Transistor #(.\type ("n")) transistor_365 (.in(1'b0), .out(L_64_e6cb4ce5), .gate(not_8_out));
  Transistor #(.\type ("n")) transistor_366 (.in(1'b0), .out(L_63_0a5e7e38), .gate(L_T0_5a901129));
  Transistor #(.\type ("n")) transistor_367 (.in(1'b0), .out(L_64_e6cb4ce5), .gate(L_T0_5a901129));
  Pull_Resistor #(.pull(1)) pull_resistor_66 (.node(L_65_6a42b4dc));
  Transistor #(.\type ("n")) transistor_368 (.in(1'b0), .out(L_65_6a42b4dc), .gate(not_2_out));
  Transistor #(.\type ("n")) transistor_369 (.in(1'b0), .out(L_65_6a42b4dc), .gate(L_T0_5a901129));
  Pull_Resistor #(.pull(1)) pull_resistor_67 (.node(L_66_3306dbdf));
  Transistor #(.\type ("n")) transistor_370 (.in(1'b0), .out(L_66_3306dbdf), .gate(or_1_out));
  Transistor #(.\type ("n")) transistor_371 (.in(1'b0), .out(L_66_3306dbdf), .gate(not_3_out));
  Transistor #(.\type ("n")) transistor_372 (.in(1'b0), .out(L_66_3306dbdf), .gate(IR4));
  Transistor #(.\type ("n")) transistor_373 (.in(1'b0), .out(L_66_3306dbdf), .gate(not_5_out));
  Transistor #(.\type ("n")) transistor_374 (.in(1'b0), .out(L_66_3306dbdf), .gate(IR2));
  Transistor #(.\type ("n")) transistor_375 (.in(1'b0), .out(L_66_3306dbdf), .gate(IR6));
  Transistor #(.\type ("n")) transistor_376 (.in(1'b0), .out(L_66_3306dbdf), .gate(not_8_out));
  Transistor #(.\type ("n")) transistor_377 (.in(1'b0), .out(L_66_3306dbdf), .gate(L_T0_5a901129));
  Pull_Resistor #(.pull(1)) pull_resistor_68 (.node(L_67_7ef59d0e));
  Pull_Resistor #(.pull(1)) pull_resistor_69 (.node(L_68_820561b0));
  Transistor #(.\type ("n")) transistor_378 (.in(1'b0), .out(L_67_7ef59d0e), .gate(not_1_out));
  Transistor #(.\type ("n")) transistor_379 (.in(1'b0), .out(L_68_820561b0), .gate(not_1_out));
  Transistor #(.\type ("n")) transistor_380 (.in(1'b0), .out(L_67_7ef59d0e), .gate(IR7));
  Transistor #(.\type ("n")) transistor_381 (.in(1'b0), .out(L_68_820561b0), .gate(not_3_out));
  Transistor #(.\type ("n")) transistor_382 (.in(1'b0), .out(L_67_7ef59d0e), .gate(IR4));
  Transistor #(.\type ("n")) transistor_383 (.in(1'b0), .out(L_68_820561b0), .gate(IR4));
  Transistor #(.\type ("n")) transistor_384 (.in(1'b0), .out(L_67_7ef59d0e), .gate(not_5_out));
  Transistor #(.\type ("n")) transistor_385 (.in(1'b0), .out(L_68_820561b0), .gate(not_5_out));
  Transistor #(.\type ("n")) transistor_386 (.in(1'b0), .out(L_67_7ef59d0e), .gate(IR2));
  Transistor #(.\type ("n")) transistor_387 (.in(1'b0), .out(L_68_820561b0), .gate(IR2));
  Transistor #(.\type ("n")) transistor_388 (.in(1'b0), .out(L_68_820561b0), .gate(IR6));
  Transistor #(.\type ("n")) transistor_389 (.in(1'b0), .out(L_68_820561b0), .gate(not_8_out));
  Transistor #(.\type ("n")) transistor_390 (.in(1'b0), .out(L_67_7ef59d0e), .gate(L_T0_5a901129));
  Transistor #(.\type ("n")) transistor_391 (.in(1'b0), .out(L_68_820561b0), .gate(L_T0_5a901129));
  Pull_Resistor #(.pull(1)) pull_resistor_70 (.node(L_69_cbdecb8a));
  Transistor #(.\type ("n")) transistor_392 (.in(1'b0), .out(L_69_cbdecb8a), .gate(or_1_out));
  Transistor #(.\type ("n")) transistor_393 (.in(1'b0), .out(L_69_cbdecb8a), .gate(IR7));
  Transistor #(.\type ("n")) transistor_394 (.in(1'b0), .out(L_69_cbdecb8a), .gate(IR4));
  Transistor #(.\type ("n")) transistor_395 (.in(1'b0), .out(L_69_cbdecb8a), .gate(not_6_out));
  Transistor #(.\type ("n")) transistor_396 (.in(1'b0), .out(L_69_cbdecb8a), .gate(IR6));
  Transistor #(.\type ("n")) transistor_397 (.in(1'b0), .out(L_69_cbdecb8a), .gate(not_8_out));
  Transistor #(.\type ("n")) transistor_398 (.in(1'b0), .out(L_69_cbdecb8a), .gate(L_T0_5a901129));
  Pull_Resistor #(.pull(1)) pull_resistor_71 (.node(L_70_099188dc));
  Transistor #(.\type ("n")) transistor_399 (.in(1'b0), .out(L_70_099188dc), .gate(not_2_out));
  Transistor #(.\type ("n")) transistor_400 (.in(1'b0), .out(L_70_099188dc), .gate(IR7));
  Transistor #(.\type ("n")) transistor_401 (.in(1'b0), .out(L_70_099188dc), .gate(IR6));
  Transistor #(.\type ("n")) transistor_402 (.in(1'b0), .out(L_70_099188dc), .gate(not_8_out));
  Transistor #(.\type ("n")) transistor_403 (.in(1'b0), .out(L_70_099188dc), .gate(L_T0_5a901129));
  Pull_Resistor #(.pull(1)) pull_resistor_72 (.node(L_71_facae7ec));
  Pull_Resistor #(.pull(1)) pull_resistor_73 (.node(L_72_92460769));
  Transistor #(.\type ("n")) transistor_404 (.in(1'b0), .out(L_72_92460769), .gate(L_T5_89b31bc6));
  Transistor #(.\type ("n")) transistor_405 (.in(1'b0), .out(L_71_facae7ec), .gate(L_T4_d9b6e407));
  Transistor #(.\type ("n")) transistor_406 (.in(1'b0), .out(L_72_92460769), .gate(not_2_out));
  Transistor #(.\type ("n")) transistor_407 (.in(1'b0), .out(L_71_facae7ec), .gate(not_4_out));
  Transistor #(.\type ("n")) transistor_408 (.in(1'b0), .out(L_72_92460769), .gate(not_4_out));
  Transistor #(.\type ("n")) transistor_409 (.in(1'b0), .out(L_72_92460769), .gate(IR3));
  Transistor #(.\type ("n")) transistor_410 (.in(1'b0), .out(L_71_facae7ec), .gate(not_5_out));
  Transistor #(.\type ("n")) transistor_411 (.in(1'b0), .out(L_72_92460769), .gate(IR2));
  Pull_Resistor #(.pull(1)) pull_resistor_74 (.node(L_73_3c19a6e4));
  Transistor #(.\type ("n")) transistor_412 (.in(1'b0), .out(L_73_3c19a6e4), .gate(or_1_out));
  Transistor #(.\type ("n")) transistor_413 (.in(1'b0), .out(L_73_3c19a6e4), .gate(not_4_out));
  Transistor #(.\type ("n")) transistor_414 (.in(1'b0), .out(L_73_3c19a6e4), .gate(IR3));
  Transistor #(.\type ("n")) transistor_415 (.in(1'b0), .out(L_73_3c19a6e4), .gate(IR2));
  Transistor #(.\type ("n")) transistor_416 (.in(1'b0), .out(L_73_3c19a6e4), .gate(L_T0_5a901129));
  Pull_Resistor #(.pull(1)) pull_resistor_75 (.node(L_74_b252c222));
  Pull_Resistor #(.pull(1)) pull_resistor_76 (.node(L_75_7b13a6b0));
  Transistor #(.\type ("n")) transistor_417 (.in(1'b0), .out(L_74_b252c222), .gate(L_T2_37fe4d42));
  Transistor #(.\type ("n")) transistor_418 (.in(1'b0), .out(L_75_7b13a6b0), .gate(not_1_out));
  Transistor #(.\type ("n")) transistor_419 (.in(1'b0), .out(L_74_b252c222), .gate(or_1_out));
  Transistor #(.\type ("n")) transistor_420 (.in(1'b0), .out(L_74_b252c222), .gate(IR7));
  Transistor #(.\type ("n")) transistor_421 (.in(1'b0), .out(L_75_7b13a6b0), .gate(IR7));
  Transistor #(.\type ("n")) transistor_422 (.in(1'b0), .out(L_74_b252c222), .gate(IR4));
  Transistor #(.\type ("n")) transistor_423 (.in(1'b0), .out(L_75_7b13a6b0), .gate(IR4));
  Transistor #(.\type ("n")) transistor_424 (.in(1'b0), .out(L_74_b252c222), .gate(not_5_out));
  Transistor #(.\type ("n")) transistor_425 (.in(1'b0), .out(L_75_7b13a6b0), .gate(not_5_out));
  Transistor #(.\type ("n")) transistor_426 (.in(1'b0), .out(L_74_b252c222), .gate(IR2));
  Transistor #(.\type ("n")) transistor_427 (.in(1'b0), .out(L_75_7b13a6b0), .gate(IR2));
  Transistor #(.\type ("n")) transistor_428 (.in(1'b0), .out(L_74_b252c222), .gate(not_7_out));
  Transistor #(.\type ("n")) transistor_429 (.in(1'b0), .out(L_75_7b13a6b0), .gate(not_7_out));
  Transistor #(.\type ("n")) transistor_430 (.in(1'b0), .out(L_74_b252c222), .gate(IR5));
  Transistor #(.\type ("n")) transistor_431 (.in(1'b0), .out(L_75_7b13a6b0), .gate(L_T0_5a901129));
  Pull_Resistor #(.pull(1)) pull_resistor_77 (.node(L_76_ea80c3c2));
  Transistor #(.\type ("n")) transistor_432 (.in(1'b0), .out(L_76_ea80c3c2), .gate(not_1_out));
  Transistor #(.\type ("n")) transistor_433 (.in(1'b0), .out(L_76_ea80c3c2), .gate(IR7));
  Transistor #(.\type ("n")) transistor_434 (.in(1'b0), .out(L_76_ea80c3c2), .gate(not_7_out));
  Pull_Resistor #(.pull(1)) pull_resistor_78 (.node(L_77_f96dcb28));
  Transistor #(.\type ("n")) transistor_435 (.in(1'b0), .out(L_77_f96dcb28), .gate(L_T2_37fe4d42));
  Transistor #(.\type ("n")) transistor_436 (.in(1'b0), .out(L_77_f96dcb28), .gate(or_1_out));
  Transistor #(.\type ("n")) transistor_437 (.in(1'b0), .out(L_77_f96dcb28), .gate(IR7));
  Transistor #(.\type ("n")) transistor_438 (.in(1'b0), .out(L_77_f96dcb28), .gate(IR4));
  Transistor #(.\type ("n")) transistor_439 (.in(1'b0), .out(L_77_f96dcb28), .gate(IR3));
  Transistor #(.\type ("n")) transistor_440 (.in(1'b0), .out(L_77_f96dcb28), .gate(IR2));
  Transistor #(.\type ("n")) transistor_441 (.in(1'b0), .out(L_77_f96dcb28), .gate(IR6));
  Transistor #(.\type ("n")) transistor_442 (.in(1'b0), .out(L_77_f96dcb28), .gate(IR5));
  Pull_Resistor #(.pull(1)) pull_resistor_79 (.node(L_78_8a0d457e));
  Pull_Resistor #(.pull(1)) pull_resistor_80 (.node(L_79_7d8df45e));
  Transistor #(.\type ("n")) transistor_443 (.in(1'b0), .out(L_78_8a0d457e), .gate(L_T3_3fe619b3));
  Transistor #(.\type ("n")) transistor_444 (.in(1'b0), .out(L_78_8a0d457e), .gate(or_1_out));
  Transistor #(.\type ("n")) transistor_445 (.in(1'b0), .out(L_79_7d8df45e), .gate(not_2_out));
  Transistor #(.\type ("n")) transistor_446 (.in(1'b0), .out(L_78_8a0d457e), .gate(IR7));
  Transistor #(.\type ("n")) transistor_447 (.in(1'b0), .out(L_79_7d8df45e), .gate(not_3_out));
  Transistor #(.\type ("n")) transistor_448 (.in(1'b0), .out(L_78_8a0d457e), .gate(IR4));
  Transistor #(.\type ("n")) transistor_449 (.in(1'b0), .out(L_78_8a0d457e), .gate(IR3));
  Transistor #(.\type ("n")) transistor_450 (.in(1'b0), .out(L_78_8a0d457e), .gate(IR2));
  Transistor #(.\type ("n")) transistor_451 (.in(1'b0), .out(L_78_8a0d457e), .gate(IR6));
  Transistor #(.\type ("n")) transistor_452 (.in(1'b0), .out(L_79_7d8df45e), .gate(IR6));
  Transistor #(.\type ("n")) transistor_453 (.in(1'b0), .out(L_79_7d8df45e), .gate(IR5));
  Transistor #(.\type ("n")) transistor_454 (.in(1'b0), .out(L_78_8a0d457e), .gate(not_8_out));
  Pull_Resistor #(.pull(1)) pull_resistor_81 (.node(L_80_053c0a7a));
  Transistor #(.\type ("n")) transistor_455 (.in(1'b0), .out(L_80_053c0a7a), .gate(L_T2_37fe4d42));
  Transistor #(.\type ("n")) transistor_456 (.in(1'b0), .out(L_80_053c0a7a), .gate(or_1_out));
  Transistor #(.\type ("n")) transistor_457 (.in(1'b0), .out(L_80_053c0a7a), .gate(not_4_out));
  Transistor #(.\type ("n")) transistor_458 (.in(1'b0), .out(L_80_053c0a7a), .gate(IR3));
  Transistor #(.\type ("n")) transistor_459 (.in(1'b0), .out(L_80_053c0a7a), .gate(IR2));
  Pull_Resistor #(.pull(1)) pull_resistor_82 (.node(L_81_2726249e));
  Transistor #(.\type ("n")) transistor_460 (.in(1'b0), .out(L_81_2726249e), .gate(L_T2_37fe4d42));
  Transistor #(.\type ("n")) transistor_461 (.in(1'b0), .out(L_81_2726249e), .gate(IR3));
  Transistor #(.\type ("n")) transistor_462 (.in(1'b0), .out(L_81_2726249e), .gate(not_6_out));
  Pull_Resistor #(.pull(1)) pull_resistor_83 (.node(L_82_298ac22b));
  Pull_Resistor #(.pull(1)) pull_resistor_84 (.node(L_83_79a418b7));
  Transistor #(.\type ("n")) transistor_463 (.in(1'b0), .out(L_82_298ac22b), .gate(L_T2_37fe4d42));
  Transistor #(.\type ("n")) transistor_464 (.in(1'b0), .out(L_83_79a418b7), .gate(L_T2_37fe4d42));
  Transistor #(.\type ("n")) transistor_465 (.in(1'b0), .out(L_82_298ac22b), .gate(not_2_out));
  Transistor #(.\type ("n")) transistor_466 (.in(1'b0), .out(L_82_298ac22b), .gate(IR3));
  Transistor #(.\type ("n")) transistor_467 (.in(1'b0), .out(L_83_79a418b7), .gate(not_5_out));
  Transistor #(.\type ("n")) transistor_468 (.in(1'b0), .out(L_82_298ac22b), .gate(IR2));
  Pull_Resistor #(.pull(1)) pull_resistor_85 (.node(L_84_e79a1766));
  Transistor #(.\type ("n")) transistor_469 (.in(1'b0), .out(L_84_e79a1766), .gate(L_T5_89b31bc6));
  Transistor #(.\type ("n")) transistor_470 (.in(1'b0), .out(L_84_e79a1766), .gate(or_1_out));
  Transistor #(.\type ("n")) transistor_471 (.in(1'b0), .out(L_84_e79a1766), .gate(IR7));
  Transistor #(.\type ("n")) transistor_472 (.in(1'b0), .out(L_84_e79a1766), .gate(IR4));
  Transistor #(.\type ("n")) transistor_473 (.in(1'b0), .out(L_84_e79a1766), .gate(IR3));
  Transistor #(.\type ("n")) transistor_474 (.in(1'b0), .out(L_84_e79a1766), .gate(IR2));
  Transistor #(.\type ("n")) transistor_475 (.in(1'b0), .out(L_84_e79a1766), .gate(not_7_out));
  Transistor #(.\type ("n")) transistor_476 (.in(1'b0), .out(L_84_e79a1766), .gate(not_8_out));
  Pull_Resistor #(.pull(1)) pull_resistor_86 (.node(L_85_b2daf010));
  Transistor #(.\type ("n")) transistor_477 (.in(1'b0), .out(L_85_b2daf010), .gate(L_T4_d9b6e407));
  Pull_Resistor #(.pull(1)) pull_resistor_87 (.node(L_86_b98cc819));
  Pull_Resistor #(.pull(1)) pull_resistor_88 (.node(L_87_c637b311));
  Transistor #(.\type ("n")) transistor_478 (.in(1'b0), .out(L_86_b98cc819), .gate(L_T3_3fe619b3));
  Transistor #(.\type ("n")) transistor_479 (.in(1'b0), .out(L_87_c637b311), .gate(or_1_out));
  Transistor #(.\type ("n")) transistor_480 (.in(1'b0), .out(L_87_c637b311), .gate(IR7));
  Transistor #(.\type ("n")) transistor_481 (.in(1'b0), .out(L_87_c637b311), .gate(IR4));
  Transistor #(.\type ("n")) transistor_482 (.in(1'b0), .out(L_87_c637b311), .gate(IR3));
  Transistor #(.\type ("n")) transistor_483 (.in(1'b0), .out(L_87_c637b311), .gate(IR2));
  Transistor #(.\type ("n")) transistor_484 (.in(1'b0), .out(L_87_c637b311), .gate(IR5));
  Transistor #(.\type ("n")) transistor_485 (.in(1'b0), .out(L_87_c637b311), .gate(L_T0_5a901129));
  Pull_Resistor #(.pull(1)) pull_resistor_89 (.node(L_88_055bb603));
  Transistor #(.\type ("n")) transistor_486 (.in(1'b0), .out(L_88_055bb603), .gate(or_1_out));
  Transistor #(.\type ("n")) transistor_487 (.in(1'b0), .out(L_88_055bb603), .gate(IR7));
  Transistor #(.\type ("n")) transistor_488 (.in(1'b0), .out(L_88_055bb603), .gate(IR4));
  Transistor #(.\type ("n")) transistor_489 (.in(1'b0), .out(L_88_055bb603), .gate(not_5_out));
  Transistor #(.\type ("n")) transistor_490 (.in(1'b0), .out(L_88_055bb603), .gate(not_6_out));
  Transistor #(.\type ("n")) transistor_491 (.in(1'b0), .out(L_88_055bb603), .gate(not_7_out));
  Transistor #(.\type ("n")) transistor_492 (.in(1'b0), .out(L_88_055bb603), .gate(L_T0_5a901129));
  Pull_Resistor #(.pull(1)) pull_resistor_90 (.node(L_89_5d5fe4c7));
  Transistor #(.\type ("n")) transistor_493 (.in(1'b0), .out(L_89_5d5fe4c7), .gate(L_T5_89b31bc6));
  Transistor #(.\type ("n")) transistor_494 (.in(1'b0), .out(L_89_5d5fe4c7), .gate(not_2_out));
  Transistor #(.\type ("n")) transistor_495 (.in(1'b0), .out(L_89_5d5fe4c7), .gate(IR4));
  Transistor #(.\type ("n")) transistor_496 (.in(1'b0), .out(L_89_5d5fe4c7), .gate(IR3));
  Transistor #(.\type ("n")) transistor_497 (.in(1'b0), .out(L_89_5d5fe4c7), .gate(IR2));
  Pull_Resistor #(.pull(1)) pull_resistor_91 (.node(L_90_55afaa76));
  Transistor #(.\type ("n")) transistor_498 (.in(1'b0), .out(L_90_55afaa76), .gate(L_T3_3fe619b3));
  Transistor #(.\type ("n")) transistor_499 (.in(1'b0), .out(L_90_55afaa76), .gate(not_5_out));
  Pull_Resistor #(.pull(1)) pull_resistor_92 (.node(L_91_d03b9369));
  Transistor #(.\type ("n")) transistor_500 (.in(1'b0), .out(L_91_d03b9369), .gate(L_T4_d9b6e407));
  Transistor #(.\type ("n")) transistor_501 (.in(1'b0), .out(L_91_d03b9369), .gate(not_2_out));
  Transistor #(.\type ("n")) transistor_502 (.in(1'b0), .out(L_91_d03b9369), .gate(not_4_out));
  Transistor #(.\type ("n")) transistor_503 (.in(1'b0), .out(L_91_d03b9369), .gate(IR3));
  Transistor #(.\type ("n")) transistor_504 (.in(1'b0), .out(L_91_d03b9369), .gate(IR2));
  Pull_Resistor #(.pull(1)) pull_resistor_93 (.node(L_92_0cc1d36a));
  Transistor #(.\type ("n")) transistor_505 (.in(1'b0), .out(L_92_0cc1d36a), .gate(L_T3_3fe619b3));
  Transistor #(.\type ("n")) transistor_506 (.in(1'b0), .out(L_92_0cc1d36a), .gate(not_4_out));
  Transistor #(.\type ("n")) transistor_507 (.in(1'b0), .out(L_92_0cc1d36a), .gate(not_5_out));
  Pull_Resistor #(.pull(1)) pull_resistor_94 (.node(L_93_eaf60893));
  Pull_Resistor #(.pull(1)) pull_resistor_95 (.node(L_94_95326b03));
  Transistor #(.\type ("n")) transistor_508 (.in(1'b0), .out(L_93_eaf60893), .gate(L_T3_3fe619b3));
  Transistor #(.\type ("n")) transistor_509 (.in(1'b0), .out(L_93_eaf60893), .gate(or_1_out));
  Transistor #(.\type ("n")) transistor_510 (.in(1'b0), .out(L_94_95326b03), .gate(or_1_out));
  Transistor #(.\type ("n")) transistor_511 (.in(1'b0), .out(L_94_95326b03), .gate(IR7));
  Transistor #(.\type ("n")) transistor_512 (.in(1'b0), .out(L_94_95326b03), .gate(IR4));
  Transistor #(.\type ("n")) transistor_513 (.in(1'b0), .out(L_93_eaf60893), .gate(not_4_out));
  Transistor #(.\type ("n")) transistor_514 (.in(1'b0), .out(L_93_eaf60893), .gate(IR3));
  Transistor #(.\type ("n")) transistor_515 (.in(1'b0), .out(L_94_95326b03), .gate(IR3));
  Transistor #(.\type ("n")) transistor_516 (.in(1'b0), .out(L_93_eaf60893), .gate(IR2));
  Transistor #(.\type ("n")) transistor_517 (.in(1'b0), .out(L_94_95326b03), .gate(IR2));
  Transistor #(.\type ("n")) transistor_518 (.in(1'b0), .out(L_94_95326b03), .gate(IR5));
  Pull_Resistor #(.pull(1)) pull_resistor_96 (.node(L_95_f060a0fd));
  Transistor #(.\type ("n")) transistor_519 (.in(1'b0), .out(L_95_f060a0fd), .gate(or_1_out));
  Transistor #(.\type ("n")) transistor_520 (.in(1'b0), .out(L_95_f060a0fd), .gate(IR7));
  Transistor #(.\type ("n")) transistor_521 (.in(1'b0), .out(L_95_f060a0fd), .gate(IR4));
  Transistor #(.\type ("n")) transistor_522 (.in(1'b0), .out(L_95_f060a0fd), .gate(IR3));
  Transistor #(.\type ("n")) transistor_523 (.in(1'b0), .out(L_95_f060a0fd), .gate(IR2));
  Transistor #(.\type ("n")) transistor_524 (.in(1'b0), .out(L_95_f060a0fd), .gate(IR6));
  Transistor #(.\type ("n")) transistor_525 (.in(1'b0), .out(L_95_f060a0fd), .gate(not_8_out));
  Pull_Resistor #(.pull(1)) pull_resistor_97 (.node(L_96_3d015798));
  Transistor #(.\type ("n")) transistor_526 (.in(1'b0), .out(L_96_3d015798), .gate(or_1_out));
  Transistor #(.\type ("n")) transistor_527 (.in(1'b0), .out(L_96_3d015798), .gate(IR7));
  Transistor #(.\type ("n")) transistor_528 (.in(1'b0), .out(L_96_3d015798), .gate(IR4));
  Transistor #(.\type ("n")) transistor_529 (.in(1'b0), .out(L_96_3d015798), .gate(not_5_out));
  Transistor #(.\type ("n")) transistor_530 (.in(1'b0), .out(L_96_3d015798), .gate(not_6_out));
  Transistor #(.\type ("n")) transistor_531 (.in(1'b0), .out(L_96_3d015798), .gate(not_7_out));
  Pull_Resistor #(.pull(1)) pull_resistor_98 (.node(L_97_f3e813cd));
  Transistor #(.\type ("n")) transistor_532 (.in(1'b0), .out(L_97_f3e813cd), .gate(not_3_out));
  Transistor #(.\type ("n")) transistor_533 (.in(1'b0), .out(L_97_f3e813cd), .gate(IR6));
  Transistor #(.\type ("n")) transistor_534 (.in(1'b0), .out(L_97_f3e813cd), .gate(IR5));
  Pull_Resistor #(.pull(1)) pull_resistor_99 (.node(L_98_f4cee2ae));
  Transistor #(.\type ("n")) transistor_535 (.in(1'b0), .out(L_98_f4cee2ae), .gate(L_T4_d9b6e407));
  Transistor #(.\type ("n")) transistor_536 (.in(1'b0), .out(L_98_f4cee2ae), .gate(or_1_out));
  Transistor #(.\type ("n")) transistor_537 (.in(1'b0), .out(L_98_f4cee2ae), .gate(IR7));
  Transistor #(.\type ("n")) transistor_538 (.in(1'b0), .out(L_98_f4cee2ae), .gate(IR4));
  Transistor #(.\type ("n")) transistor_539 (.in(1'b0), .out(L_98_f4cee2ae), .gate(IR3));
  Transistor #(.\type ("n")) transistor_540 (.in(1'b0), .out(L_98_f4cee2ae), .gate(IR2));
  Transistor #(.\type ("n")) transistor_541 (.in(1'b0), .out(L_98_f4cee2ae), .gate(IR6));
  Transistor #(.\type ("n")) transistor_542 (.in(1'b0), .out(L_98_f4cee2ae), .gate(IR5));
  Pull_Resistor #(.pull(1)) pull_resistor_100 (.node(L_99_bb939962));
  Pull_Resistor #(.pull(1)) pull_resistor_101 (.node(L_100_16b00339));
  Transistor #(.\type ("n")) transistor_543 (.in(1'b0), .out(L_99_bb939962), .gate(L_T2_37fe4d42));
  Transistor #(.\type ("n")) transistor_544 (.in(1'b0), .out(L_100_16b00339), .gate(L_T2_37fe4d42));
  Transistor #(.\type ("n")) transistor_545 (.in(1'b0), .out(L_99_bb939962), .gate(or_1_out));
  Transistor #(.\type ("n")) transistor_546 (.in(1'b0), .out(L_100_16b00339), .gate(or_1_out));
  Transistor #(.\type ("n")) transistor_547 (.in(1'b0), .out(L_99_bb939962), .gate(IR7));
  Transistor #(.\type ("n")) transistor_548 (.in(1'b0), .out(L_100_16b00339), .gate(IR7));
  Transistor #(.\type ("n")) transistor_549 (.in(1'b0), .out(L_99_bb939962), .gate(IR4));
  Transistor #(.\type ("n")) transistor_550 (.in(1'b0), .out(L_100_16b00339), .gate(IR4));
  Transistor #(.\type ("n")) transistor_551 (.in(1'b0), .out(L_99_bb939962), .gate(not_5_out));
  Transistor #(.\type ("n")) transistor_552 (.in(1'b0), .out(L_100_16b00339), .gate(not_5_out));
  Transistor #(.\type ("n")) transistor_553 (.in(1'b0), .out(L_99_bb939962), .gate(IR2));
  Transistor #(.\type ("n")) transistor_554 (.in(1'b0), .out(L_100_16b00339), .gate(IR2));
  Transistor #(.\type ("n")) transistor_555 (.in(1'b0), .out(L_99_bb939962), .gate(IR6));
  Transistor #(.\type ("n")) transistor_556 (.in(1'b0), .out(L_99_bb939962), .gate(IR5));
  Transistor #(.\type ("n")) transistor_557 (.in(1'b0), .out(L_100_16b00339), .gate(IR5));
  Pull_Resistor #(.pull(1)) pull_resistor_102 (.node(L_101_c09bb9ac));
  Transistor #(.\type ("n")) transistor_558 (.in(1'b0), .out(L_101_c09bb9ac), .gate(L_T4_d9b6e407));
  Transistor #(.\type ("n")) transistor_559 (.in(1'b0), .out(L_101_c09bb9ac), .gate(or_1_out));
  Transistor #(.\type ("n")) transistor_560 (.in(1'b0), .out(L_101_c09bb9ac), .gate(IR7));
  Transistor #(.\type ("n")) transistor_561 (.in(1'b0), .out(L_101_c09bb9ac), .gate(IR4));
  Transistor #(.\type ("n")) transistor_562 (.in(1'b0), .out(L_101_c09bb9ac), .gate(not_5_out));
  Transistor #(.\type ("n")) transistor_563 (.in(1'b0), .out(L_101_c09bb9ac), .gate(not_6_out));
  Transistor #(.\type ("n")) transistor_564 (.in(1'b0), .out(L_101_c09bb9ac), .gate(not_7_out));
  Pull_Resistor #(.pull(1)) pull_resistor_103 (.node(L_102_614a85bf));
  Transistor #(.\type ("n")) transistor_565 (.in(1'b0), .out(L_102_614a85bf), .gate(L_T5_89b31bc6));
  Transistor #(.\type ("n")) transistor_566 (.in(1'b0), .out(L_102_614a85bf), .gate(or_1_out));
  Transistor #(.\type ("n")) transistor_567 (.in(1'b0), .out(L_102_614a85bf), .gate(IR7));
  Transistor #(.\type ("n")) transistor_568 (.in(1'b0), .out(L_102_614a85bf), .gate(IR4));
  Transistor #(.\type ("n")) transistor_569 (.in(1'b0), .out(L_102_614a85bf), .gate(IR3));
  Transistor #(.\type ("n")) transistor_570 (.in(1'b0), .out(L_102_614a85bf), .gate(IR2));
  Transistor #(.\type ("n")) transistor_571 (.in(1'b0), .out(L_102_614a85bf), .gate(not_7_out));
  Pull_Resistor #(.pull(1)) pull_resistor_104 (.node(L_103_52940b9a));
  Transistor #(.\type ("n")) transistor_572 (.in(1'b0), .out(L_103_52940b9a), .gate(L_T5_89b31bc6));
  Transistor #(.\type ("n")) transistor_573 (.in(1'b0), .out(L_103_52940b9a), .gate(or_1_out));
  Transistor #(.\type ("n")) transistor_574 (.in(1'b0), .out(L_103_52940b9a), .gate(IR7));
  Transistor #(.\type ("n")) transistor_575 (.in(1'b0), .out(L_103_52940b9a), .gate(IR4));
  Transistor #(.\type ("n")) transistor_576 (.in(1'b0), .out(L_103_52940b9a), .gate(IR3));
  Transistor #(.\type ("n")) transistor_577 (.in(1'b0), .out(L_103_52940b9a), .gate(IR2));
  Transistor #(.\type ("n")) transistor_578 (.in(1'b0), .out(L_103_52940b9a), .gate(IR6));
  Transistor #(.\type ("n")) transistor_579 (.in(1'b0), .out(L_103_52940b9a), .gate(not_8_out));
  Pull_Resistor #(.pull(1)) pull_resistor_105 (.node(L_104_443c5ff0));
  Pull_Resistor #(.pull(1)) pull_resistor_106 (.node(L_105_5ce959fd));
  Transistor #(.\type ("n")) transistor_580 (.in(1'b0), .out(L_105_5ce959fd), .gate(L_T3_3fe619b3));
  Transistor #(.\type ("n")) transistor_581 (.in(1'b0), .out(L_104_443c5ff0), .gate(L_T2_37fe4d42));
  Transistor #(.\type ("n")) transistor_582 (.in(1'b0), .out(L_104_443c5ff0), .gate(or_1_out));
  Transistor #(.\type ("n")) transistor_583 (.in(1'b0), .out(L_105_5ce959fd), .gate(or_1_out));
  Transistor #(.\type ("n")) transistor_584 (.in(1'b0), .out(L_104_443c5ff0), .gate(IR7));
  Transistor #(.\type ("n")) transistor_585 (.in(1'b0), .out(L_105_5ce959fd), .gate(IR7));
  Transistor #(.\type ("n")) transistor_586 (.in(1'b0), .out(L_104_443c5ff0), .gate(IR4));
  Transistor #(.\type ("n")) transistor_587 (.in(1'b0), .out(L_105_5ce959fd), .gate(IR4));
  Transistor #(.\type ("n")) transistor_588 (.in(1'b0), .out(L_104_443c5ff0), .gate(not_5_out));
  Transistor #(.\type ("n")) transistor_589 (.in(1'b0), .out(L_105_5ce959fd), .gate(not_5_out));
  Transistor #(.\type ("n")) transistor_590 (.in(1'b0), .out(L_105_5ce959fd), .gate(IR2));
  Transistor #(.\type ("n")) transistor_591 (.in(1'b0), .out(L_104_443c5ff0), .gate(not_6_out));
  Transistor #(.\type ("n")) transistor_592 (.in(1'b0), .out(L_104_443c5ff0), .gate(not_7_out));
  Transistor #(.\type ("n")) transistor_593 (.in(1'b0), .out(L_104_443c5ff0), .gate(IR5));
  Transistor #(.\type ("n")) transistor_594 (.in(1'b0), .out(L_105_5ce959fd), .gate(not_8_out));
  Pull_Resistor #(.pull(1)) pull_resistor_107 (.node(L_106_2a9581c6));
  Transistor #(.\type ("n")) transistor_595 (.in(1'b0), .out(L_106_2a9581c6), .gate(not_1_out));
  Transistor #(.\type ("n")) transistor_596 (.in(1'b0), .out(L_106_2a9581c6), .gate(not_7_out));
  Pull_Resistor #(.pull(1)) pull_resistor_108 (.node(L_107_a96ffaba));
  Transistor #(.\type ("n")) transistor_597 (.in(1'b0), .out(L_107_a96ffaba), .gate(not_1_out));
  Transistor #(.\type ("n")) transistor_598 (.in(1'b0), .out(L_107_a96ffaba), .gate(IR7));
  Transistor #(.\type ("n")) transistor_599 (.in(1'b0), .out(L_107_a96ffaba), .gate(IR6));
  Pull_Resistor #(.pull(1)) pull_resistor_109 (.node(L_108_c205b5ff));
  Transistor #(.\type ("n")) transistor_600 (.in(1'b0), .out(L_108_c205b5ff), .gate(or_1_out));
  Transistor #(.\type ("n")) transistor_601 (.in(1'b0), .out(L_108_c205b5ff), .gate(IR7));
  Transistor #(.\type ("n")) transistor_602 (.in(1'b0), .out(L_108_c205b5ff), .gate(not_4_out));
  Transistor #(.\type ("n")) transistor_603 (.in(1'b0), .out(L_108_c205b5ff), .gate(IR2));
  Transistor #(.\type ("n")) transistor_604 (.in(1'b0), .out(L_108_c205b5ff), .gate(not_7_out));
  Transistor #(.\type ("n")) transistor_605 (.in(1'b0), .out(L_108_c205b5ff), .gate(L_T0_5a901129));
  Pull_Resistor #(.pull(1)) pull_resistor_110 (.node(L_109_2fe88a94));
  Transistor #(.\type ("n")) transistor_606 (.in(1'b0), .out(L_109_2fe88a94), .gate(or_1_out));
  Transistor #(.\type ("n")) transistor_607 (.in(1'b0), .out(L_109_2fe88a94), .gate(IR7));
  Transistor #(.\type ("n")) transistor_608 (.in(1'b0), .out(L_109_2fe88a94), .gate(IR4));
  Transistor #(.\type ("n")) transistor_609 (.in(1'b0), .out(L_109_2fe88a94), .gate(not_6_out));
  Transistor #(.\type ("n")) transistor_610 (.in(1'b0), .out(L_109_2fe88a94), .gate(IR6));
  Transistor #(.\type ("n")) transistor_611 (.in(1'b0), .out(L_109_2fe88a94), .gate(not_8_out));
  Transistor #(.\type ("n")) transistor_612 (.in(1'b0), .out(L_109_2fe88a94), .gate(L_T1X_624de7e6));
  Pull_Resistor #(.pull(1)) pull_resistor_111 (.node(L_110_4cc555bd));
  Pull_Resistor #(.pull(1)) pull_resistor_112 (.node(L_111_2b81c3c9));
  Transistor #(.\type ("n")) transistor_613 (.in(1'b0), .out(L_111_2b81c3c9), .gate(L_T3_3fe619b3));
  Transistor #(.\type ("n")) transistor_614 (.in(1'b0), .out(L_110_4cc555bd), .gate(or_1_out));
  Transistor #(.\type ("n")) transistor_615 (.in(1'b0), .out(L_110_4cc555bd), .gate(IR7));
  Transistor #(.\type ("n")) transistor_616 (.in(1'b0), .out(L_110_4cc555bd), .gate(not_4_out));
  Transistor #(.\type ("n")) transistor_617 (.in(1'b0), .out(L_111_2b81c3c9), .gate(not_4_out));
  Transistor #(.\type ("n")) transistor_618 (.in(1'b0), .out(L_111_2b81c3c9), .gate(IR3));
  Transistor #(.\type ("n")) transistor_619 (.in(1'b0), .out(L_110_4cc555bd), .gate(not_5_out));
  Transistor #(.\type ("n")) transistor_620 (.in(1'b0), .out(L_110_4cc555bd), .gate(IR2));
  Transistor #(.\type ("n")) transistor_621 (.in(1'b0), .out(L_111_2b81c3c9), .gate(not_6_out));
  Transistor #(.\type ("n")) transistor_622 (.in(1'b0), .out(L_110_4cc555bd), .gate(IR6));
  Transistor #(.\type ("n")) transistor_623 (.in(1'b0), .out(L_110_4cc555bd), .gate(L_T0_5a901129));
  Pull_Resistor #(.pull(1)) pull_resistor_113 (.node(L_112_708a0f10));
  Transistor #(.\type ("n")) transistor_624 (.in(1'b0), .out(L_112_708a0f10), .gate(not_2_out));
  Transistor #(.\type ("n")) transistor_625 (.in(1'b0), .out(L_112_708a0f10), .gate(not_7_out));
  Transistor #(.\type ("n")) transistor_626 (.in(1'b0), .out(L_112_708a0f10), .gate(not_8_out));
  Transistor #(.\type ("n")) transistor_627 (.in(1'b0), .out(L_112_708a0f10), .gate(L_T1X_624de7e6));
  Pull_Resistor #(.pull(1)) pull_resistor_114 (.node(L_113_fbaa75ad));
  Transistor #(.\type ("n")) transistor_628 (.in(1'b0), .out(L_113_fbaa75ad), .gate(or_1_out));
  Transistor #(.\type ("n")) transistor_629 (.in(1'b0), .out(L_113_fbaa75ad), .gate(IR7));
  Transistor #(.\type ("n")) transistor_630 (.in(1'b0), .out(L_113_fbaa75ad), .gate(IR4));
  Transistor #(.\type ("n")) transistor_631 (.in(1'b0), .out(L_113_fbaa75ad), .gate(not_6_out));
  Transistor #(.\type ("n")) transistor_632 (.in(1'b0), .out(L_113_fbaa75ad), .gate(IR6));
  Transistor #(.\type ("n")) transistor_633 (.in(1'b0), .out(L_113_fbaa75ad), .gate(not_8_out));
  Transistor #(.\type ("n")) transistor_634 (.in(1'b0), .out(L_113_fbaa75ad), .gate(L_T0_5a901129));
  Pull_Resistor #(.pull(1)) pull_resistor_115 (.node(L_114_f9625e87));
  Pull_Resistor #(.pull(1)) pull_resistor_116 (.node(L_115_b1986fe2));
  Transistor #(.\type ("n")) transistor_635 (.in(1'b0), .out(L_115_b1986fe2), .gate(L_T4_d9b6e407));
  Transistor #(.\type ("n")) transistor_636 (.in(1'b0), .out(L_114_f9625e87), .gate(or_1_out));
  Transistor #(.\type ("n")) transistor_637 (.in(1'b0), .out(L_115_b1986fe2), .gate(or_1_out));
  Transistor #(.\type ("n")) transistor_638 (.in(1'b0), .out(L_114_f9625e87), .gate(IR7));
  Transistor #(.\type ("n")) transistor_639 (.in(1'b0), .out(L_115_b1986fe2), .gate(IR7));
  Transistor #(.\type ("n")) transistor_640 (.in(1'b0), .out(L_114_f9625e87), .gate(IR4));
  Transistor #(.\type ("n")) transistor_641 (.in(1'b0), .out(L_115_b1986fe2), .gate(IR4));
  Transistor #(.\type ("n")) transistor_642 (.in(1'b0), .out(L_115_b1986fe2), .gate(IR3));
  Transistor #(.\type ("n")) transistor_643 (.in(1'b0), .out(L_114_f9625e87), .gate(not_5_out));
  Transistor #(.\type ("n")) transistor_644 (.in(1'b0), .out(L_114_f9625e87), .gate(IR2));
  Transistor #(.\type ("n")) transistor_645 (.in(1'b0), .out(L_115_b1986fe2), .gate(IR2));
  Transistor #(.\type ("n")) transistor_646 (.in(1'b0), .out(L_114_f9625e87), .gate(IR6));
  Transistor #(.\type ("n")) transistor_647 (.in(1'b0), .out(L_115_b1986fe2), .gate(not_7_out));
  Transistor #(.\type ("n")) transistor_648 (.in(1'b0), .out(L_115_b1986fe2), .gate(IR5));
  Transistor #(.\type ("n")) transistor_649 (.in(1'b0), .out(L_114_f9625e87), .gate(not_8_out));
  Transistor #(.\type ("n")) transistor_650 (.in(1'b0), .out(L_114_f9625e87), .gate(L_T0_5a901129));
  Pull_Resistor #(.pull(1)) pull_resistor_117 (.node(L_116_0ba24dc4));
  Transistor #(.\type ("n")) transistor_651 (.in(1'b0), .out(L_116_0ba24dc4), .gate(not_2_out));
  Transistor #(.\type ("n")) transistor_652 (.in(1'b0), .out(L_116_0ba24dc4), .gate(not_3_out));
  Transistor #(.\type ("n")) transistor_653 (.in(1'b0), .out(L_116_0ba24dc4), .gate(not_7_out));
  Transistor #(.\type ("n")) transistor_654 (.in(1'b0), .out(L_116_0ba24dc4), .gate(IR5));
  Transistor #(.\type ("n")) transistor_655 (.in(1'b0), .out(L_116_0ba24dc4), .gate(L_T1X_624de7e6));
  Pull_Resistor #(.pull(1)) pull_resistor_118 (.node(L_117_10a3c8b1));
  Transistor #(.\type ("n")) transistor_656 (.in(1'b0), .out(L_117_10a3c8b1), .gate(or_1_out));
  Transistor #(.\type ("n")) transistor_657 (.in(1'b0), .out(L_117_10a3c8b1), .gate(not_3_out));
  Transistor #(.\type ("n")) transistor_658 (.in(1'b0), .out(L_117_10a3c8b1), .gate(IR4));
  Transistor #(.\type ("n")) transistor_659 (.in(1'b0), .out(L_117_10a3c8b1), .gate(not_5_out));
  Transistor #(.\type ("n")) transistor_660 (.in(1'b0), .out(L_117_10a3c8b1), .gate(not_6_out));
  Transistor #(.\type ("n")) transistor_661 (.in(1'b0), .out(L_117_10a3c8b1), .gate(not_7_out));
  Transistor #(.\type ("n")) transistor_662 (.in(1'b0), .out(L_117_10a3c8b1), .gate(L_T1X_624de7e6));
  Pull_Resistor #(.pull(1)) pull_resistor_119 (.node(L_118_e0e8abfe));
  Pull_Resistor #(.pull(1)) pull_resistor_120 (.node(L_119_86db347d));
  Transistor #(.\type ("n")) transistor_663 (.in(1'b0), .out(L_118_e0e8abfe), .gate(not_1_out));
  Transistor #(.\type ("n")) transistor_664 (.in(1'b0), .out(L_119_86db347d), .gate(or_1_out));
  Transistor #(.\type ("n")) transistor_665 (.in(1'b0), .out(L_118_e0e8abfe), .gate(IR7));
  Transistor #(.\type ("n")) transistor_666 (.in(1'b0), .out(L_119_86db347d), .gate(not_3_out));
  Transistor #(.\type ("n")) transistor_667 (.in(1'b0), .out(L_118_e0e8abfe), .gate(IR4));
  Transistor #(.\type ("n")) transistor_668 (.in(1'b0), .out(L_119_86db347d), .gate(IR4));
  Transistor #(.\type ("n")) transistor_669 (.in(1'b0), .out(L_119_86db347d), .gate(IR3));
  Transistor #(.\type ("n")) transistor_670 (.in(1'b0), .out(L_118_e0e8abfe), .gate(not_5_out));
  Transistor #(.\type ("n")) transistor_671 (.in(1'b0), .out(L_118_e0e8abfe), .gate(IR2));
  Transistor #(.\type ("n")) transistor_672 (.in(1'b0), .out(L_118_e0e8abfe), .gate(IR6));
  Transistor #(.\type ("n")) transistor_673 (.in(1'b0), .out(L_119_86db347d), .gate(not_7_out));
  Transistor #(.\type ("n")) transistor_674 (.in(1'b0), .out(L_118_e0e8abfe), .gate(L_T1X_624de7e6));
  Transistor #(.\type ("n")) transistor_675 (.in(1'b0), .out(L_119_86db347d), .gate(L_T1X_624de7e6));
  Pull_Resistor #(.pull(1)) pull_resistor_121 (.node(L_120_c53a083f));
  Pull_Resistor #(.pull(1)) pull_resistor_122 (.node(L_121_da158f44));
  Transistor #(.\type ("n")) transistor_676 (.in(1'b0), .out(L_120_c53a083f), .gate(or_1_out));
  Transistor #(.\type ("n")) transistor_677 (.in(1'b0), .out(L_120_c53a083f), .gate(not_3_out));
  Transistor #(.\type ("n")) transistor_678 (.in(1'b0), .out(L_120_c53a083f), .gate(not_4_out));
  Transistor #(.\type ("n")) transistor_679 (.in(1'b0), .out(L_120_c53a083f), .gate(not_5_out));
  Transistor #(.\type ("n")) transistor_680 (.in(1'b0), .out(L_120_c53a083f), .gate(IR2));
  Transistor #(.\type ("n")) transistor_681 (.in(1'b0), .out(L_121_da158f44), .gate(IR6));
  Transistor #(.\type ("n")) transistor_682 (.in(1'b0), .out(L_120_c53a083f), .gate(not_7_out));
  Transistor #(.\type ("n")) transistor_683 (.in(1'b0), .out(L_120_c53a083f), .gate(L_T0_5a901129));
  Pull_Resistor #(.pull(1)) pull_resistor_123 (.node(L_122_0e8f1988));
  Transistor #(.\type ("n")) transistor_684 (.in(1'b0), .out(L_122_0e8f1988), .gate(L_T3_3fe619b3));
  Transistor #(.\type ("n")) transistor_685 (.in(1'b0), .out(L_122_0e8f1988), .gate(IR4));
  Transistor #(.\type ("n")) transistor_686 (.in(1'b0), .out(L_122_0e8f1988), .gate(not_5_out));
  Transistor #(.\type ("n")) transistor_687 (.in(1'b0), .out(L_122_0e8f1988), .gate(not_6_out));
  Pull_Resistor #(.pull(1)) pull_resistor_124 (.node(L_123_a8638cda));
  Transistor #(.\type ("n")) transistor_688 (.in(1'b0), .out(L_123_a8638cda), .gate(L_T2_37fe4d42));
  Transistor #(.\type ("n")) transistor_689 (.in(1'b0), .out(L_123_a8638cda), .gate(IR4));
  Transistor #(.\type ("n")) transistor_690 (.in(1'b0), .out(L_123_a8638cda), .gate(IR3));
  Transistor #(.\type ("n")) transistor_691 (.in(1'b0), .out(L_123_a8638cda), .gate(not_6_out));
  Pull_Resistor #(.pull(1)) pull_resistor_125 (.node(L_124_8d81fffd));
  Pull_Resistor #(.pull(1)) pull_resistor_126 (.node(L_125_8f968e43));
  Transistor #(.\type ("n")) transistor_692 (.in(1'b0), .out(L_124_8d81fffd), .gate(L_T5_89b31bc6));
  Transistor #(.\type ("n")) transistor_693 (.in(1'b0), .out(L_125_8f968e43), .gate(L_T4_d9b6e407));
  Transistor #(.\type ("n")) transistor_694 (.in(1'b0), .out(L_124_8d81fffd), .gate(not_2_out));
  Transistor #(.\type ("n")) transistor_695 (.in(1'b0), .out(L_125_8f968e43), .gate(not_4_out));
  Transistor #(.\type ("n")) transistor_696 (.in(1'b0), .out(L_124_8d81fffd), .gate(IR3));
  Transistor #(.\type ("n")) transistor_697 (.in(1'b0), .out(L_125_8f968e43), .gate(not_5_out));
  Transistor #(.\type ("n")) transistor_698 (.in(1'b0), .out(L_124_8d81fffd), .gate(IR2));
  Pull_Resistor #(.pull(1)) pull_resistor_127 (.node(L_126_7e3003c6));
  Transistor #(.\type ("n")) transistor_699 (.in(1'b0), .out(L_126_7e3003c6), .gate(IR7));
  Pull_Resistor #(.pull(1)) pull_resistor_128 (.node(L_127_28942974));
  Transistor #(.\type ("n")) transistor_700 (.in(1'b0), .out(L_127_28942974), .gate(or_1_out));
  Transistor #(.\type ("n")) transistor_701 (.in(1'b0), .out(L_127_28942974), .gate(not_3_out));
  Transistor #(.\type ("n")) transistor_702 (.in(1'b0), .out(L_127_28942974), .gate(not_4_out));
  Transistor #(.\type ("n")) transistor_703 (.in(1'b0), .out(L_127_28942974), .gate(not_5_out));
  Transistor #(.\type ("n")) transistor_704 (.in(1'b0), .out(L_127_28942974), .gate(IR2));
  Transistor #(.\type ("n")) transistor_705 (.in(1'b0), .out(L_127_28942974), .gate(IR6));
  Transistor #(.\type ("n")) transistor_706 (.in(1'b0), .out(L_127_28942974), .gate(not_8_out));
  Pull_Resistor #(.pull(1)) pull_resistor_129 (.node(L_128_23d7200b));
  Pull_Resistor #(.pull(1)) pull_resistor_130 (.node(L_129_7b5e5edf));
  Transistor #(.\type ("n")) transistor_707 (.in(1'b0), .out(L_128_23d7200b), .gate(IR0));
  Transistor #(.\type ("n")) transistor_708 (.in(1'b0), .out(L_129_7b5e5edf), .gate(or_1_out));
  Transistor #(.\type ("n")) transistor_709 (.in(1'b0), .out(L_129_7b5e5edf), .gate(IR7));
  Transistor #(.\type ("n")) transistor_710 (.in(1'b0), .out(L_129_7b5e5edf), .gate(IR4));
  Transistor #(.\type ("n")) transistor_711 (.in(1'b0), .out(L_128_23d7200b), .gate(not_5_out));
  Transistor #(.\type ("n")) transistor_712 (.in(1'b0), .out(L_129_7b5e5edf), .gate(not_5_out));
  Transistor #(.\type ("n")) transistor_713 (.in(1'b0), .out(L_128_23d7200b), .gate(IR2));
  Transistor #(.\type ("n")) transistor_714 (.in(1'b0), .out(L_129_7b5e5edf), .gate(IR2));

  // Notes on the sheet:
  //   TODO: Move IR0 to random logic
endmodule

module PREDECODE (
  input  PHI2,
  input  L_0_IR_c32b8001,
  input  D0,
  input  D1,
  input  D2,
  input  D3,
  input  D4,
  input  D5,
  input  D6,
  input  D7,
  output L_IMPLIED_b029c4af,
  output L_TWOCYCLE_54b4f369,
  output L_PD0_ff4f5362,
  output L_PD1_2bbb5f50,
  output L_PD2_b780aebe,
  output L_PD3_595d30b7,
  output L_PD4_d7b0250f,
  output L_PD5_1b763385,
  output L_PD6_cacfa412,
  output L_PD7_1b7e0f3f
);

  wire and1_out, and2_out, and3_out, and4_out, and5_out, and6_out, and7_out, and8_out, d_latch_1_not_q,
       d_latch_2_not_q, d_latch_3_not_q, d_latch_4_not_q, d_latch_5_not_q, d_latch_6_not_q, d_latch_7_not_q,
       d_latch_8_not_q, nand1_out, nor1_out, nor2_out, nor3_out, nor4_out, nor5_out, not_1_out, not_2_out,
       not_3_out, not_4_out, not_5_out, not_6_out, not_7_out, not_8_out, not_9_out, not_10_out, not_11_out,
       not_12_out, not_13_out, not_22_out;

  not not_1 (not_1_out, D0);
  not not_2 (not_2_out, D1);
  not not_3 (not_3_out, D2);
  not not_4 (not_4_out, D3);
  not not_5 (not_5_out, D4);
  not not_6 (not_6_out, D5);
  not not_7 (not_7_out, D6);
  not not_8 (not_8_out, D7);
  not not_9 (not_9_out, L_0_IR_c32b8001);
  D_Latch d_latch_1 (.NOT_Q(d_latch_1_not_q), .D(not_1_out), .EN(PHI2));  // open: Q
  D_Latch d_latch_2 (.NOT_Q(d_latch_2_not_q), .D(not_2_out), .EN(PHI2));  // open: Q
  D_Latch d_latch_3 (.NOT_Q(d_latch_3_not_q), .D(not_3_out), .EN(PHI2));  // open: Q
  D_Latch d_latch_4 (.NOT_Q(d_latch_4_not_q), .D(not_4_out), .EN(PHI2));  // open: Q
  D_Latch d_latch_5 (.NOT_Q(d_latch_5_not_q), .D(not_5_out), .EN(PHI2));  // open: Q
  D_Latch d_latch_6 (.NOT_Q(d_latch_6_not_q), .D(not_6_out), .EN(PHI2));  // open: Q
  D_Latch d_latch_7 (.NOT_Q(d_latch_7_not_q), .D(not_7_out), .EN(PHI2));  // open: Q
  D_Latch d_latch_8 (.NOT_Q(d_latch_8_not_q), .D(not_8_out), .EN(PHI2));  // open: Q
  and and1 (and1_out, d_latch_1_not_q, not_9_out);
  and and2 (and2_out, d_latch_2_not_q, not_9_out);
  and and3 (and3_out, d_latch_3_not_q, not_9_out);
  and and4 (and4_out, d_latch_4_not_q, not_9_out);
  and and5 (and5_out, d_latch_5_not_q, not_9_out);
  and and6 (and6_out, d_latch_6_not_q, not_9_out);
  and and7 (and7_out, d_latch_7_not_q, not_9_out);
  and and8 (and8_out, d_latch_8_not_q, not_9_out);
  not not_10 (not_10_out, and4_out);
  nor nor1 (nor1_out, and1_out, and3_out, not_10_out);
  nor nor2 (nor2_out, and2_out, and5_out, and8_out);
  not not_11 (not_11_out, and1_out);
  not not_12 (not_12_out, and4_out);
  nor nor3 (nor3_out, not_11_out, and3_out, not_12_out, and5_out);
  not not_13 (not_13_out, and8_out);
  nor nor4 (nor4_out, and1_out, not_13_out);
  not not_14 (L_PD0_ff4f5362, and1_out);
  not not_15 (L_PD1_2bbb5f50, and2_out);
  not not_16 (L_PD2_b780aebe, and3_out);
  not not_17 (L_PD3_595d30b7, and4_out);
  not not_18 (L_PD4_d7b0250f, and5_out);
  not not_19 (L_PD5_1b763385, and6_out);
  not not_20 (L_PD6_cacfa412, and7_out);
  not not_21 (L_PD7_1b7e0f3f, and8_out);
  not not_22 (not_22_out, nor2_out);
  nand nand1 (nand1_out, nor1_out, not_22_out);
  nor nor5 (nor5_out, nor3_out, nor4_out);
  not not_23 (L_IMPLIED_b029c4af, nor1_out);
  and and9 (L_TWOCYCLE_54b4f369, nand1_out, nor5_out);
endmodule

module RANDOM_LOGIC (
  input  PHI1,
  input  X0,
  input  X1,
  input  X2,
  input  X3,
  input  X4,
  input  X5,
  input  X6,
  input  X7,
  input  X8,
  input  X9,
  input  X10,
  input  X11,
  input  X12,
  input  X13,
  input  X14,
  input  X15,
  input  X16,
  input  X17,
  input  X18,
  input  X19,
  input  X20,
  input  X21,
  input  X22,
  input  X23,
  input  X24,
  input  X25,
  input  X26,
  input  X27,
  input  X28,
  input  X29,
  input  X30,
  input  X31,
  input  X32,
  input  X33,
  input  X34,
  input  X35,
  input  X36,
  input  X37,
  input  X38,
  input  X39,
  input  X40,
  input  X41,
  input  X42,
  input  X43,
  input  X44,
  input  X45,
  input  X46,
  input  X47,
  input  X48,
  input  X49,
  input  X50,
  input  X51,
  input  X52,
  input  X53,
  input  X54,
  input  X55,
  input  X56,
  input  X57,
  input  X58,
  input  X59,
  input  X60,
  input  X61,
  input  X62,
  input  X63,
  input  X64,
  input  X65,
  input  X66,
  input  X67,
  input  X68,
  input  X69,
  input  X70,
  input  X71,
  input  X72,
  input  X73,
  input  X74,
  input  X75,
  input  X76,
  input  X77,
  input  X78,
  input  X79,
  input  X80,
  input  X81,
  input  X82,
  input  X83,
  input  X84,
  input  X85,
  input  X86,
  input  X87,
  input  X88,
  input  X89,
  input  X90,
  input  X91,
  input  X92,
  input  X93,
  input  X94,
  input  X95,
  input  X96,
  input  X97,
  input  X98,
  input  X99,
  input  X100,
  input  X101,
  input  X102,
  input  X103,
  input  X104,
  input  X105,
  input  X106,
  input  X107,
  input  X108,
  input  X109,
  input  X110,
  input  X111,
  input  X112,
  input  X113,
  input  X114,
  input  X115,
  input  X116,
  input  X117,
  input  X118,
  input  X119,
  input  X120,
  input  X121,
  input  X122,
  input  X123,
  input  X124,
  input  X125,
  input  X126,
  input  X127,
  input  X128,
  input  X129,
  input  PHI2,
  input  L_IR5_9e15d54c,
  input  L_NMIP_021a4ca5,
  input  RESP,
  input  L_IRQP_c24e1171,
  input  AVR,
  input  ACR,
  input  SO,
  input  L_TWOCYCLE_54b4f369,
  input  L_IMPLIED_b029c4af,
  input  RDY,
  input  in_143,
  input  DB6,
  input  DB5,
  input  in_146,
  input  DB3,
  input  in_148,
  input  DB1,
  input  in_150,
  output FETCH,
  output L_T0_5a901129,
  output L_T2_37fe4d42,
  output L_T3_3fe619b3,
  output L_T4_d9b6e407,
  output L_T5_89b31bc6,
  output L_0_ADL0_f8fabdab,
  output L_0_ADL1_4e9a6ca8,
  output L_0_ADL2_2c4a79f4,
  output Y_SB_d628d28f,
  output X_SB_222038db,
  output SB_Y_9a33ae5e,
  output SB_X_cf392641,
  output S_SB_e37affed,
  output S_ADL_07acd992,
  output SB_S_4c94ee46,
  output S_S_09f08a69,
  output L_V_OUT_959779aa,
  output L_I_OUT_6792f219,
  output L_D_OUT_7d61c6e7,
  output L_C_OUT_f91ece9c,
  output L_N_OUT_10df9d15,
  output L_Z_OUT_2813b2ba,
  output NDB_ADD_ee0a1870,
  output DB_ADD_48d85b7e,
  output L_0_ADD_81d17e61,
  output SB_ADD_0eab26ac,
  output ADL_ADD_e28b8a30,
  output ANDS,
  output EORS,
  output ORS,
  output L_ACIN_e173f520,
  output SUMS,
  output L_DAA_82b80d94,
  output ADD_SB7_a8f4b77a,
  output ADD_SB06_a3738230,
  output ADD_ADL_3fac4345,
  output L_DSA_ea96e89b,
  output SRS,
  output DL_ADL_6c5e0116,
  output DL_DB_69522204,
  output DL_ADH_3839a3d0,
  output ADH_ABH_8f72aca9,
  output ADL_ABL_5bea59e2,
  output SB_AC_b159eec5,
  output AC_SB_c49f602a,
  output L_0_ADH0_e340c71e,
  output L_0_ADH17_f181a8fa,
  output AC_DB_519ce409,
  output SB_DB_641efa5a,
  output SB_ADH_4f1456ff,
  output ADL_PCL_9a95c372,
  output PCL_PCL_4f350f4d,
  output PCH_ADH_ead93594,
  output PCL_ADL_ee043dbc,
  output PCH_DB_a81fefa0,
  output PCL_DB_4172714e,
  output ADH_PCH_61520abf,
  output PCH_PCH_807b9fbd,
  output TRESX,
  output L_0_IR_c32b8001,
  output ENDS,
  output ENDX,
  output TRES1,
  output T1,
  output L_T1X_624de7e6,
  output RD,
  output R_W_47630a0a,
  output L_1_PC_f2b91046,
  output P_DB_42279b60,
  output IR5_I_e7eeeda5,
  output IR5_C_8cbf3e52,
  output IR5_D_ec89b364,
  output L_0_V_f0a8dd83,
  output ACR_C_5cb02b46,
  output DBZ_Z_a7859eb1,
  output DB_N_68ba26fc,
  output DB_P_37e5c1ba,
  output DB_C_01ed158e,
  output DB_V_92adf01b,
  output WR,
  output DB7,
  output out_233,
  output out_234,
  output DB4,
  output out_236,
  output DB2,
  output out_238,
  output DB0
);

  wire alu_setup_1_and, alu_setup_1_inc_sb, alu_setup_1_sr, branch_logic_1_brfw,
       branch_logic_1_l_brtaken_ace66327, BRK6E, bus_control_1_pgx, bus_control_1_ztst, dispatch_1_acrl2,
       dispatch_1_stor, dispatch_1_tres2, INTERRUPT_RESET_CONTROL_b_out, INTERRUPT_RESET_CONTROL_brk7,
       INTERRUPT_RESET_CONTROL_dores, INTERRUPT_RESET_CONTROL_l_donmi_29470de9, L_READY_a37d69a3,
       pc_setup_1_dl_pch_0dc37cb4, pc_setup_1_l_adl_pcl_a2520980, pc_setup_1_l_pch_pch_e0d9e687,
       pc_setup_1_pc_db_a835deaa, regs_control_1_sbxy, regs_control_1_stkop, regs_control_1_stxy, T0, T5, T6;

  INT_RESET_CONTROL INTERRUPT_RESET_CONTROL (
    .B_OUT(INTERRUPT_RESET_CONTROL_b_out), .BRK6E(BRK6E), .BRK7(INTERRUPT_RESET_CONTROL_brk7),
    .DORES(INTERRUPT_RESET_CONTROL_dores), .L_DONMI_29470de9(INTERRUPT_RESET_CONTROL_l_donmi_29470de9),
    .BR2(X80), .T0(T0), .BRK5(X22), .L_IRQP_c24e1171(L_IRQP_c24e1171), .L_I_OUT_6792f219(L_I_OUT_6792f219),
    .L_READY_a37d69a3(L_READY_a37d69a3), .PHI1(PHI1), .RESP(RESP), .PHI2(PHI2),
    .L_NMIP_021a4ca5(L_NMIP_021a4ca5));
  INT_VECTOR INTERRUPT_VECTOR (
    .L_0_ADL0_f8fabdab(L_0_ADL0_f8fabdab), .L_0_ADL1_4e9a6ca8(L_0_ADL1_4e9a6ca8),
    .L_0_ADL2_2c4a79f4(L_0_ADL2_2c4a79f4), .PHI2(PHI2), .BRK5(X22), .BRK7(INTERRUPT_RESET_CONTROL_brk7),
    .DORES(INTERRUPT_RESET_CONTROL_dores), .L_DONMI_29470de9(INTERRUPT_RESET_CONTROL_l_donmi_29470de9));
  REGS_CONTROL regs_control_1 (
    .S_ADL_07acd992(S_ADL_07acd992), .Y_SB_d628d28f(Y_SB_d628d28f), .STXY(regs_control_1_stxy),
    .X_SB_222038db(X_SB_222038db), .S_SB_e37affed(S_SB_e37affed), .SB_X_cf392641(SB_X_cf392641),
    .SBXY(regs_control_1_sbxy), .SB_Y_9a33ae5e(SB_Y_9a33ae5e), .SB_S_4c94ee46(SB_S_4c94ee46),
    .S_S_09f08a69(S_S_09f08a69), .STKOP(regs_control_1_stkop), .STOR(dispatch_1_stor), .D35(X35),
    .L_0_090b2452(X0), .L_1_28cbbb7d(X1), .in_6(X2), .L_3_39a566ac(X3), .in_8(X4), .L_5_9518e519(X5),
    .L_6_5b7e39b9(X6), .L_7_14ab2533(X7), .L_8_05eb4f56(X8), .PHI1(PHI1), .L_9_0082242d(X9),
    .L_10_57b0d741(X10), .in_15(X11), .L_12_85a3418f(X12), .in_17(X13), .in_18(X14), .L_15_5dad5732(X15),
    .L_16_c7396848(X16), ._12(X17), .L_18_4ab117a9(X18), .PHI2(PHI2), .L_19_e094c090(X19),
    .L_20_adeacd1b(X20), .L_21_ada5c31c(X21), .L_22_f545d19e(X22), .L_23_d0835dd9(X23), .L_24_b6efc2f4(X24),
    .L_25_f5ad6aee(X25), .L_26_ffeee2da(X26), .L_48_330a6f3f(X48), .L_READY_a37d69a3(L_READY_a37d69a3));
  FLAGS flags_1 (
    .out_28(DB0), .DB1(out_238), .DB2(DB2), .out_31(out_236), .DB4(DB4), .DB5(out_234), .out_34(out_233),
    .out_35(DB7), .L_Z_OUT_2813b2ba(L_Z_OUT_2813b2ba), .L_N_OUT_10df9d15(L_N_OUT_10df9d15),
    .L_C_OUT_f91ece9c(L_C_OUT_f91ece9c), .L_D_OUT_7d61c6e7(L_D_OUT_7d61c6e7),
    .L_I_OUT_6792f219(L_I_OUT_6792f219), .L_V_OUT_959779aa(L_V_OUT_959779aa),
    .L_IR5_9e15d54c(L_IR5_9e15d54c), .DB0(in_150), .IR5_I_e7eeeda5(IR5_I_e7eeeda5), .AVR(AVR),
    .DB_V_92adf01b(DB_V_92adf01b), .D112(X112), .L_0_V_f0a8dd83(L_0_V_f0a8dd83), .in_4(DB1), .SO(SO),
    .in_5(in_148), .DB3(DB3), .in_7(in_146), .P_DB_42279b60(P_DB_42279b60), .in_8(DB5), .DB6(DB6),
    .DB7(in_143), .DB_P_37e5c1ba(DB_P_37e5c1ba), .DBZ_Z_a7859eb1(DBZ_Z_a7859eb1),
    .DB_N_68ba26fc(DB_N_68ba26fc), .IR5_C_8cbf3e52(IR5_C_8cbf3e52), .ACR(ACR),
    .B_OUT(INTERRUPT_RESET_CONTROL_b_out), .DB_C_01ed158e(DB_C_01ed158e), .ACR_C_5cb02b46(ACR_C_5cb02b46),
    .IR5_D_ec89b364(IR5_D_ec89b364), .PHI1(PHI1), .PHI2(PHI2));
  ALU_SETUP alu_setup_1 (
    .ADD_SB06_a3738230(ADD_SB06_a3738230), .ADD_ADL_3fac4345(ADD_ADL_3fac4345),
    .L_DSA_ea96e89b(L_DSA_ea96e89b), .INC_SB(alu_setup_1_inc_sb), .SR(alu_setup_1_sr),
    .DB_ADD_48d85b7e(DB_ADD_48d85b7e), .L_0_ADD_81d17e61(L_0_ADD_81d17e61),
    .SB_ADD_0eab26ac(SB_ADD_0eab26ac), .ADL_ADD_e28b8a30(ADL_ADD_e28b8a30), .AND(alu_setup_1_and),
    .ANDS(ANDS), .EORS(EORS), .ORS(ORS), .L_ACIN_e173f520(L_ACIN_e173f520), .SRS(SRS), .SUMS(SUMS),
    .L_DAA_82b80d94(L_DAA_82b80d94), .NDB_ADD_ee0a1870(NDB_ADD_ee0a1870),
    .ADD_SB7_a8f4b77a(ADD_SB7_a8f4b77a), .D56(X56), .D69(X69), .D70(X70),
    .L_READY_a37d69a3(L_READY_a37d69a3), .D75(X75), .D76(X76), .D84(X84), .D85(X85), .D86(X86), .D87(X87),
    .D88(X88), .D89(X89), .T0(T0), .T1(T1), .BRK6E(BRK6E), .T5(T5), .T6(T6), .PGX(bus_control_1_pgx),
    .BR3(X93), .L_D_OUT_7d61c6e7(L_D_OUT_7d61c6e7), .L_C_OUT_f91ece9c(L_C_OUT_f91ece9c),
    .STKOP(regs_control_1_stkop), .PHI1(PHI1), .D26(X26), .D27(X27), .D29(X29), .D30(X30), .D31(X31),
    .D32(X32), .D33(X33), .D34(X34), .D35(X35), .D36(X36), .PHI2(PHI2), .D37(X37), .D38(X38), .D39(X39),
    .D40(X40), .D41(X41), .D42(X42), .D43(X43), .D44(X44), .D45(X45), .D47(X47), .BRFW(branch_logic_1_brfw),
    .D48(X48), .D49(X49), .D50(X50), .D51(X51), .D52(X52), .D53(X53), .D54(X54));
  BUS_CONTROL bus_control_1 (
    .ADH_ABH_8f72aca9(ADH_ABH_8f72aca9), .L_0_ADH0_e340c71e(L_0_ADH0_e340c71e),
    .DL_DB_69522204(DL_DB_69522204), .L_0_ADH17_f181a8fa(L_0_ADH17_f181a8fa),
    .SB_AC_b159eec5(SB_AC_b159eec5), .ZTST(bus_control_1_ztst), .ADL_ABL_5bea59e2(ADL_ABL_5bea59e2),
    .AC_SB_c49f602a(AC_SB_c49f602a), .SB_DB_641efa5a(SB_DB_641efa5a), .AC_DB_519ce409(AC_DB_519ce409),
    .PGX(bus_control_1_pgx), .SB_ADH_4f1456ff(SB_ADH_4f1456ff), .DL_ADH_3839a3d0(DL_ADH_3839a3d0),
    .DL_ADL_6c5e0116(DL_ADL_6c5e0116), .D129(X129), .L_0_ADL0_f8fabdab(L_0_ADL0_f8fabdab), .BR2(X80),
    .ACRL2(dispatch_1_acrl2), .D55(X55), .DL_PCH_0dc37cb4(pc_setup_1_dl_pch_0dc37cb4), .BR3(X93),
    .L_READY_a37d69a3(L_READY_a37d69a3), .T2(X28), .INC_SB(alu_setup_1_inc_sb), .D45(X45), .BRK6E(BRK6E),
    .D46(X46), .D47(X47), .D48(X48), .D57(X57), .STXY(regs_control_1_stxy), .D101(X101),
    .L_PCH_PCH_e0d9e687(pc_setup_1_l_pch_pch_e0d9e687), .T0(T0), .T1(T1), .T5(T6), .T6(T5), .D56(X56),
    .D58(X58), .PHI1(PHI1), .D59(X59), .D60(X60), .D61(X61), .D62(X62), .D63(X63), .D64(X64), .D65(X65),
    .D66(X66), .D67(X67), .D68(X68), .PHI2(PHI2), .AND(alu_setup_1_and), .D71(X71), .D72(X72), .D73(X73),
    .D74(X74), .D79(X79), .STOR(dispatch_1_stor), .D81(X81), .D82(X82), .D84(X84),
    .SBXY(regs_control_1_sbxy), .D89(X89), .D90(X90), .D91(X91), .D83(X83), .D128(X128));
  PC_SETUP pc_setup_1 (
    .PCL_DB_4172714e(PCL_DB_4172714e), .PCH_DB_a81fefa0(PCH_DB_a81fefa0),
    .PC_DB_a835deaa(pc_setup_1_pc_db_a835deaa), .PCL_ADL_ee043dbc(PCL_ADL_ee043dbc),
    .PCH_ADH_ead93594(PCH_ADH_ead93594), .PCL_PCL_4f350f4d(PCL_PCL_4f350f4d),
    .ADL_PCL_9a95c372(ADL_PCL_9a95c372), .L_ADL_PCL_a2520980(pc_setup_1_l_adl_pcl_a2520980),
    .DL_PCH_0dc37cb4(pc_setup_1_dl_pch_0dc37cb4), .ADH_PCH_61520abf(ADH_PCH_61520abf),
    .PCH_PCH_807b9fbd(PCH_PCH_807b9fbd), .L_PCH_PCH_e0d9e687(pc_setup_1_l_pch_pch_e0d9e687), .D56(X56),
    .D77(X77), .D78(X78), .D83(X83), .D84(X84), .D94(X94), .D95(X95), .D96(X96), .PHI1(PHI1), .D129(X129),
    .L_READY_a37d69a3(L_READY_a37d69a3), .BR3(X93), .BR2(X80), .T0(T0), .T1(T1), .BR0(X73), .PHI2(PHI2));
  DISPATCH dispatch_1 (
    .R_W_47630a0a(R_W_47630a0a), .WR(WR), .T1(T1), .TRES1(TRES1), .L_T0_5a901129(L_T0_5a901129), .T0(T0),
    .T5(T5), .L_T1X_624de7e6(L_T1X_624de7e6), .L_1_PC_1c371e3f(L_1_PC_f2b91046), .ACRL2(dispatch_1_acrl2),
    .T6(T6), .TRES2(dispatch_1_tres2), .TRESX(TRESX), .STOR(dispatch_1_stor), .ENDX_Debug(ENDX),
    .ENDS_Debug(ENDS), .L_0_IR_c32b8001(L_0_IR_c32b8001), .FETCH(FETCH), .L_READY_a37d69a3(L_READY_a37d69a3),
    .RD(RD), .L_BRTAKEN_ace66327(branch_logic_1_l_brtaken_ace66327),
    .L_TWOCYCLE_54b4f369(L_TWOCYCLE_54b4f369), .BRK6E(BRK6E),
    .L_ADL_PCL_a2520980(pc_setup_1_l_adl_pcl_a2520980), .L_IMPLED_6d196eb4(L_IMPLIED_b029c4af), .BR2(X80),
    .RESP(RESP), .ACR(ACR), .DORES(INTERRUPT_RESET_CONTROL_dores),
    .PC_DB_a835deaa(pc_setup_1_pc_db_a835deaa), .D91(X91), .D92(X92), .PHI1(PHI1), .BR3(X93), .D96(X96),
    .D97(X97), .D98(X98), .D100(X100), .D101(X101), .D102(X102), .D103(X103), .D104(X104), .D105(X105),
    .D106(X106), .D107(X107), .D111(X111), .PHI2(PHI2), .D122(X122), .D123(X123), .D124(X124), .D125(X125),
    .RDY(RDY), .B_OUT(INTERRUPT_RESET_CONTROL_b_out), .BRFW(branch_logic_1_brfw));
  FLAGS_CONTROL flags_control_1 (
    .IR5_I_e7eeeda5(IR5_I_e7eeeda5), .IR5_C_8cbf3e52(IR5_C_8cbf3e52), .IR5_D_ec89b364(IR5_D_ec89b364),
    .L_0_V_f0a8dd83(L_0_V_f0a8dd83), .ACR_C_5cb02b46(ACR_C_5cb02b46), .P_DB_42279b60(P_DB_42279b60),
    .DBZ_Z_a7859eb1(DBZ_Z_a7859eb1), .DB_N_68ba26fc(DB_N_68ba26fc), .DB_P_37e5c1ba(DB_P_37e5c1ba),
    .DB_C_01ed158e(DB_C_01ed158e), .DB_V_92adf01b(DB_V_92adf01b), .D99(X99), .D108(X108), .D110(X110),
    .D120(X120), .PHI2(PHI2), .D127(X127), .D107(X107), .T6(T6), .D112(X112), .D116(X116), .D117(X117),
    .D118(X118), .D119(X119), .ZTST(bus_control_1_ztst), .D109(X109), .L_READY_a37d69a3(L_READY_a37d69a3),
    .SR(alu_setup_1_sr), .D98(X98), .D114(X114), .D115(X115), .D113(X113));
  BRANCH_LOGIC branch_logic_1 (
    .L_BRTAKEN_ace66327(branch_logic_1_l_brtaken_ace66327), .BRFW(branch_logic_1_brfw), .D126(X126),
    .L_C_OUT_f91ece9c(L_C_OUT_f91ece9c), .L_V_OUT_959779aa(L_V_OUT_959779aa),
    .L_N_OUT_10df9d15(L_N_OUT_10df9d15), .L_IR5_9e15d54c(L_IR5_9e15d54c),
    .L_Z_OUT_2813b2ba(L_Z_OUT_2813b2ba), .PHI1(PHI1), .PHI2(PHI2), .DB7(in_143), .BR2(X80), .D121(X121));
  EXTENDED_CYCLE_COUNTER extended_cycle_counter_1 (
    .L_T2_37fe4d42(L_T2_37fe4d42), .L_T3_3fe619b3(L_T3_3fe619b3), .L_T4_d9b6e407(L_T4_d9b6e407),
    .L_T5_89b31bc6(L_T5_89b31bc6), .TRES2(dispatch_1_tres2), .L_READY_a37d69a3(L_READY_a37d69a3), .T1(T1),
    .PHI1(PHI1), .PHI2(PHI2));

  // Other names for the same wires on the sheet: BR0 = X73; BR2 = X80; BR3 = X93; T2 = X28

  // Notes on the sheet:
  //   BRK5
  //   BRK5
  //   JSR2
  //   STK2
  //   Push/pull
endmodule

module D_Latch (
  input  D,
  input  EN,
  output Q,
  output NOT_Q
);

  D_Flip_Flop #(.trigger("high")) d_ff_1 (.D(D), .clk(EN), .Q(Q), .Qn(NOT_Q));  // open: preset, reset
endmodule

module NMI_FF (
  input  L_NMI_35d02a51,
  input  PHI2,
  output NMIP
);

  wire and_1_out, and_2_out, nor_1_out, nor_2_out, not_1_out;

  not not_1 (not_1_out, L_NMI_35d02a51);
  and and_1 (and_1_out, not_1_out, PHI2);
  nor nor_1 (nor_1_out, and_2_out, nor_2_out);
  and and_2 (and_2_out, L_NMI_35d02a51, PHI2);
  nor nor_2 (nor_2_out, nor_1_out, and_1_out);
  not not_2 (NMIP, nor_2_out);
endmodule
module INT_RESET_CONTROL (
  input  PHI1,
  input  PHI2,
  input  BRK5,
  input  L_READY_a37d69a3,
  input  RESP,
  input  L_NMIP_021a4ca5,
  input  BR2,
  input  T0,
  input  L_IRQP_c24e1171,
  input  L_I_OUT_6792f219,
  output BRK6E,
  output BRK7,
  output DORES,
  output L_DONMI_29470de9,
  output B_OUT
);

  wire and_1_out, and_2_out, and_3_out, and_4_out, and_5_out, d_latch_1_q, d_latch_2_q, d_latch_3_q,
       d_latch_4_not_q, d_latch_5_q, d_latch_6_not_q, d_latch_7_q, d_latch_8_q, d_latch_9_q, d_latch_10_q,
       d_latch_11_q, d_latch_12_not_q, d_latch_13_q, d_latch_14_not_q, d_latch_15_q, nand_1_out, nor_1_out,
       nor_2_out, nor_3_out, nor_4_out, nor_5_out, nor_6_out, nor_7_out, nor_9_out, nor_10_out, not_1_out,
       not_2_out, not_3_out, not_4_out, not_5_out, not_6_out, not_7_out, not_8_out, or_1_out, or_2_out;

  and and_1 (and_1_out, BRK5, not_1_out);
  not not_1 (not_1_out, L_READY_a37d69a3);
  not not_2 (not_2_out, L_READY_a37d69a3);
  and and_2 (and_2_out, not_2_out, BRK6E);
  and and_3 (and_3_out, L_I_OUT_6792f219, not_3_out);
  not not_3 (not_3_out, BRK6E);
  D_Latch d_latch_1 (.Q(d_latch_1_q), .D(and_1_out), .EN(PHI2));  // open: NOT_Q
  D_Latch d_latch_2 (.Q(d_latch_2_q), .D(RESP), .EN(PHI2));  // open: NOT_Q
  D_Latch d_latch_3 (.Q(d_latch_3_q), .D(nor_5_out), .EN(PHI1));  // open: NOT_Q
  D_Latch d_latch_4 (.NOT_Q(d_latch_4_not_q), .D(BRK7), .EN(PHI2));  // open: Q
  D_Latch d_latch_5 (.Q(d_latch_5_q), .D(L_NMIP_021a4ca5), .EN(PHI1));  // open: NOT_Q
  D_Latch d_latch_6 (.NOT_Q(d_latch_6_not_q), .D(L_DONMI_29470de9), .EN(PHI2));  // open: Q
  D_Latch d_latch_7 (.Q(d_latch_7_q), .D(L_DONMI_29470de9), .EN(PHI2));  // open: NOT_Q
  D_Latch d_latch_8 (.Q(d_latch_8_q), .D(and_2_out), .EN(PHI1));  // open: NOT_Q
  not not_4 (not_4_out, and_3_out);
  D_Latch d_latch_9 (.Q(d_latch_9_q), .D(nor_10_out), .EN(PHI1));  // open: NOT_Q
  not not_5 (not_5_out, d_latch_9_q);
  not not_6 (not_6_out, d_latch_1_q);
  and and_4 (and_4_out, not_6_out, nand_1_out);
  nand nand_1 (nand_1_out, L_READY_a37d69a3, d_latch_12_not_q);
  nor nor_1 (nor_1_out, d_latch_2_q, d_latch_3_q);
  nor nor_2 (nor_2_out, d_latch_5_q, nor_7_out);
  D_Latch d_latch_10 (.Q(d_latch_10_q), .D(nor_2_out), .EN(PHI1));  // open: NOT_Q
  D_Latch d_latch_11 (.Q(d_latch_11_q), .D(d_latch_6_not_q), .EN(PHI1));  // open: NOT_Q
  nor nor_3 (nor_3_out, d_latch_7_q, d_latch_8_q);
  nor nor_4 (nor_4_out, L_IRQP_c24e1171, not_4_out);
  not not_7 (not_7_out, L_DONMI_29470de9);
  and and_5 (and_5_out, or_2_out, not_5_out);
  D_Latch d_latch_12 (.NOT_Q(d_latch_12_not_q), .D(and_4_out), .EN(PHI1));  // open: Q
  nor nor_5 (nor_5_out, nor_1_out, BRK6E);
  nor nor_6 (nor_6_out, d_latch_4_not_q, L_NMIP_021a4ca5, nor_2_out);
  nor nor_7 (nor_7_out, d_latch_10_q, d_latch_11_q);
  nor nor_8 (L_DONMI_29470de9, d_latch_15_q, nor_3_out);
  nor nor_9 (nor_9_out, BR2, T0);
  or or_1 (or_1_out, nor_4_out, not_7_out);
  not not_8 (not_8_out, or_1_out);
  D_Latch d_latch_13 (.Q(d_latch_13_q), .D(and_5_out), .EN(PHI2));  // open: NOT_Q
  not not_9 (DORES, nor_1_out);
  or or_2 (or_2_out, nor_9_out, not_8_out);
  nor nor_10 (nor_10_out, d_latch_13_q, BRK6E);
  D_Latch d_latch_14 (.NOT_Q(d_latch_14_not_q), .D(d_latch_12_not_q), .EN(PHI2));  // open: Q
  not not_10 (BRK6E, d_latch_14_not_q);
  nor nor_11 (BRK7, d_latch_12_not_q, BRK5);
  D_Latch d_latch_15 (.Q(d_latch_15_q), .D(nor_6_out), .EN(PHI1));  // open: NOT_Q
  nor nor_12 (B_OUT, DORES, nor_10_out);

  // Other names for the same wires on the sheet: L_ready_9a3f8f92 = L_READY_a37d69a3

  // Notes on the sheet:
  //   /NMIP
  //   /I_OUT
  //   /IRQP
  //   INTERRUPT CYCLE 6-7
  //   RESET FLIP/FLOP
  //   NMI EDGE DETECT
  //   INTERRUPT CHECK
  //   BR2
  //   T0
  //   B FLAG
  //   /DONMI
  //   /DONMI
endmodule

module INT_VECTOR (
  input  PHI2,
  input  BRK5,
  input  BRK7,
  input  DORES,
  input  L_DONMI_29470de9,
  output L_0_ADL0_f8fabdab,
  output L_0_ADL1_4e9a6ca8,
  output L_0_ADL2_2c4a79f4
);

  wire nor_1_out, nor_2_out, not_1_out, not_2_out, not_3_out;

  not not_1 (not_1_out, DORES);
  not not_2 (not_2_out, BRK5);
  nor nor_1 (nor_1_out, BRK7, not_1_out);
  not not_3 (not_3_out, nor_1_out);
  nor nor_2 (nor_2_out, BRK7, DORES, L_DONMI_29470de9);
  D_Latch d_latch_1 (.NOT_Q(L_0_ADL0_f8fabdab), .D(not_2_out), .EN(PHI2));  // open: Q
  D_Latch d_latch_2 (.NOT_Q(L_0_ADL1_4e9a6ca8), .D(not_3_out), .EN(PHI2));  // open: Q
  D_Latch d_latch_3 (.Q(L_0_ADL2_2c4a79f4), .D(nor_2_out), .EN(PHI2));  // open: NOT_Q

  // Notes on the sheet:
  //   FFFA:NMI, 1010
  //   FFFC:RESET, 1100
  //   FFFE:IRQ/BRK, 1110
endmodule

module REGS_CONTROL (
  input  PHI1,
  input  PHI2,
  input  STOR,
  input  L_0_090b2452,
  input  L_1_28cbbb7d,
  input  in_6,
  input  L_3_39a566ac,
  input  in_8,
  input  L_5_9518e519,
  input  L_6_5b7e39b9,
  input  L_7_14ab2533,
  input  L_8_05eb4f56,
  input  L_9_0082242d,
  input  L_10_57b0d741,
  input  in_15,
  input  L_12_85a3418f,
  input  in_17,
  input  in_18,
  input  L_15_5dad5732,
  input  L_16_c7396848,
  input  _12,
  input  L_18_4ab117a9,
  input  L_19_e094c090,
  input  L_20_adeacd1b,
  input  L_21_ada5c31c,
  input  L_22_f545d19e,
  input  L_23_d0835dd9,
  input  L_24_b6efc2f4,
  input  L_25_f5ad6aee,
  input  L_26_ffeee2da,
  input  L_48_330a6f3f,
  input  L_READY_a37d69a3,
  input  D35,
  output Y_SB_d628d28f,
  output STXY,
  output X_SB_222038db,
  output S_SB_e37affed,
  output SB_X_cf392641,
  output SBXY,
  output SB_Y_9a33ae5e,
  output SB_S_4c94ee46,
  output S_S_09f08a69,
  output STKOP,
  output S_ADL_07acd992
);

  wire and_1_out, and_2_out, and_3_out, and_4_out, and_5_out, and_6_out, buffer_1_out, buffer_2_out,
       buffer_4_out, buffer_5_out, buffer_6_out, buffer_7_out, d_latch_1_q, d_latch_2_not_q, d_latch_3_not_q,
       d_latch_4_not_q, d_latch_5_not_q, d_latch_6_not_q, d_latch_7_not_q, d_latch_8_not_q, d_latch_9_not_q,
       L_2_143403ae_out, L_4_558283f2_out, L_13_587da886_out, L_14_4f483598_out, L_17_0f5278c7_out,
       nor_1_out, nor_2_out, nor_3_out, nor_6_out, nor_7_out, nor_8_out, nor_9_out, nor_10_out, nor_11_out,
       nor_12_out, not_1_out, not_2_out, not_3_out, not_4_out;

  not not_1 (not_1_out, L_7_14ab2533);
  nor nor_1 (nor_1_out, in_18, L_15_5dad5732, L_16_c7396848);
  not not_2 (not_2_out, _12);
  nor nor_2 (nor_2_out, L_18_4ab117a9, L_19_e094c090, L_20_adeacd1b);
  not not_3 (not_3_out, L_48_330a6f3f);
  and and_1 (and_1_out, L_6_5b7e39b9, L_7_14ab2533);
  and and_2 (and_2_out, L_6_5b7e39b9, not_1_out);
  nor L_13_587da886 (L_13_587da886_out, L_21_ada5c31c, L_22_f545d19e, L_23_d0835dd9, L_24_b6efc2f4, L_25_f5ad6aee, L_26_ffeee2da);
  D_Latch d_latch_1 (.Q(d_latch_1_q), .D(L_READY_a37d69a3), .EN(PHI1));  // open: NOT_Q
  nor L_17_0f5278c7 (L_17_0f5278c7_out, not_3_out, L_READY_a37d69a3);
  nor nor_3 (nor_3_out, L_1_28cbbb7d, in_6, L_3_39a566ac, in_8, L_5_9518e519, and_1_out, and_3_out);
  and and_3 (and_3_out, L_0_090b2452, STOR);
  and and_4 (and_4_out, STOR, L_12_85a3418f);
  nor L_2_143403ae (L_2_143403ae_out, and_4_out, and_2_out, L_8_05eb4f56, L_9_0082242d, L_10_57b0d741, in_15, in_17);
  and and_5 (and_5_out, L_21_ada5c31c, d_latch_1_q);
  nor nor_4 (STKOP, L_13_587da886_out, d_latch_1_q);
  and L_4_558283f2 (L_4_558283f2_out, L_0_090b2452, STOR);
  and and_6 (and_6_out, STOR, L_12_85a3418f);
  nor nor_5 (STXY, L_4_558283f2_out, and_6_out);
  nand L_11_aa2e7fa3 (SBXY, nor_1_out, nor_2_out);
  nor nor_6 (nor_6_out, in_17, STKOP, L_17_0f5278c7_out);
  nor L_14_4f483598 (L_14_4f483598_out, and_5_out, D35);
  not not_4 (not_4_out, nor_6_out);
  D_Latch d_latch_2 (.NOT_Q(d_latch_2_not_q), .D(nor_3_out), .EN(PHI2));  // open: Q
  D_Latch d_latch_3 (.NOT_Q(d_latch_3_not_q), .D(L_2_143403ae_out), .EN(PHI2));  // open: Q
  D_Latch d_latch_4 (.NOT_Q(d_latch_4_not_q), .D(not_2_out), .EN(PHI2));  // open: Q
  D_Latch d_latch_5 (.NOT_Q(d_latch_5_not_q), .D(nor_1_out), .EN(PHI2));  // open: Q
  D_Latch d_latch_6 (.NOT_Q(d_latch_6_not_q), .D(nor_2_out), .EN(PHI2));  // open: Q
  D_Latch d_latch_7 (.NOT_Q(d_latch_7_not_q), .D(nor_6_out), .EN(PHI2));  // open: Q
  D_Latch d_latch_8 (.NOT_Q(d_latch_8_not_q), .D(not_4_out), .EN(PHI2));  // open: Q
  D_Latch d_latch_9 (.NOT_Q(d_latch_9_not_q), .D(L_14_4f483598_out), .EN(PHI2));  // open: Q
  nor nor_7 (nor_7_out, PHI2, d_latch_2_not_q);
  buf buffer_1 (buffer_1_out, nor_7_out);
  nor nor_8 (nor_8_out, PHI2, d_latch_3_not_q);
  buf buffer_2 (buffer_2_out, nor_8_out);
  buf buffer_3 (S_SB_e37affed, d_latch_4_not_q);
  nor nor_9 (nor_9_out, PHI2, d_latch_5_not_q);
  buf buffer_4 (buffer_4_out, nor_9_out);
  nor nor_10 (nor_10_out, PHI2, d_latch_6_not_q);
  buf buffer_5 (buffer_5_out, nor_10_out);
  nor nor_11 (nor_11_out, PHI2, d_latch_7_not_q);
  buf buffer_6 (buffer_6_out, nor_11_out);
  nor nor_12 (nor_12_out, PHI2, d_latch_8_not_q);
  buf buffer_7 (buffer_7_out, nor_12_out);
  buf buffer_8 (S_ADL_07acd992, d_latch_9_not_q);
  nor nor_13 (Y_SB_d628d28f, PHI2, buffer_1_out);
  nor nor_14 (X_SB_222038db, PHI2, buffer_2_out);
  nor nor_15 (SB_X_cf392641, PHI2, buffer_4_out);
  nor nor_16 (SB_Y_9a33ae5e, PHI2, buffer_5_out);
  nor nor_17 (SB_S_4c94ee46, PHI2, buffer_6_out);
  nor nor_18 (S_S_09f08a69, PHI2, buffer_7_out);

  // Notes on the sheet:
  //   JRS2
  //   3
  //   TXS
  //   #SB/X
  //   #S/SB
  //   #SB/Y
  //   15.2
  //   18
  //   STOR
  //   STOR
  //   #SB/S
  //   STKOP
  //   #S/ADL
  //   #Y/SB
  //   #X/SB
  //   #S/SB
  //   SBXY
endmodule

module ABH (
  input  PHI1,
  input  PHI2,
  input  ADH_ABH_8f72aca9,
  input  ADH0,
  input  ADH1,
  input  ADH2,
  input  ADH3,
  input  ADH4,
  input  ADH5,
  input  ADH6,
  input  ADH7,
  output A8,
  output A9,
  output A10,
  output A11,
  output A12,
  output A13,
  output A14,
  output A15
);

  ABH_BIT _0 (.Ax(A8), .ADH_ABH_8f72aca9(ADH_ABH_8f72aca9), .ADHx(ADH0), .PHI1(PHI1), .PHI2(PHI2));
  ABH_BIT _1 (.Ax(A9), .ADH_ABH_8f72aca9(ADH_ABH_8f72aca9), .ADHx(ADH1), .PHI1(PHI1), .PHI2(PHI2));
  ABH_BIT _2 (.Ax(A10), .ADH_ABH_8f72aca9(ADH_ABH_8f72aca9), .ADHx(ADH2), .PHI1(PHI1), .PHI2(PHI2));
  ABH_BIT _3 (.Ax(A11), .ADH_ABH_8f72aca9(ADH_ABH_8f72aca9), .ADHx(ADH3), .PHI1(PHI1), .PHI2(PHI2));
  ABH_BIT _4 (.Ax(A12), .ADH_ABH_8f72aca9(ADH_ABH_8f72aca9), .ADHx(ADH4), .PHI1(PHI1), .PHI2(PHI2));
  ABH_BIT _5 (.Ax(A13), .ADH_ABH_8f72aca9(ADH_ABH_8f72aca9), .ADHx(ADH5), .PHI1(PHI1), .PHI2(PHI2));
  ABH_BIT _6 (.Ax(A14), .ADH_ABH_8f72aca9(ADH_ABH_8f72aca9), .ADHx(ADH6), .PHI1(PHI1), .PHI2(PHI2));
  ABH_BIT _7 (.Ax(A15), .ADH_ABH_8f72aca9(ADH_ABH_8f72aca9), .ADHx(ADH7), .PHI1(PHI1), .PHI2(PHI2));
endmodule

module EXTENDED_CYCLE_COUNTER (
  input  PHI1,
  input  PHI2,
  input  TRES2,
  input  L_READY_a37d69a3,
  input  T1,
  output L_T2_37fe4d42,
  output L_T3_3fe619b3,
  output L_T4_d9b6e407,
  output L_T5_89b31bc6
);

  wire d_latch_1_not_q, d_latch_2_not_q, d_latch_3_q, d_latch_4_not_q, d_latch_5_q, d_latch_6_not_q,
       d_latch_7_q, d_latch_8_not_q, d_latch_9_q, multiplexer_1_out, multiplexer_2_out, multiplexer_3_out,
       multiplexer_4_out, nor_1_out, nor_2_out, nor_3_out, nor_4_out, not_5_out, undriven;

  D_Latch d_latch_1 (.NOT_Q(d_latch_1_not_q), .D(T1), .EN(PHI2));  // open: Q
  Multiplexer multiplexer_1 (
    .in0(d_latch_1_not_q), .in1(d_latch_2_not_q), .out(multiplexer_1_out), .sel(L_READY_a37d69a3));
  Multiplexer multiplexer_2 (
    .in0(d_latch_2_not_q), .in1(d_latch_4_not_q), .out(multiplexer_2_out), .sel(L_READY_a37d69a3));
  Multiplexer multiplexer_3 (
    .in0(d_latch_4_not_q), .in1(d_latch_6_not_q), .out(multiplexer_3_out), .sel(L_READY_a37d69a3));
  Multiplexer multiplexer_4 (
    .in0(d_latch_6_not_q), .in1(d_latch_8_not_q), .out(multiplexer_4_out), .sel(L_READY_a37d69a3));
  nor nor_1 (nor_1_out, TRES2, d_latch_3_q);
  nor nor_2 (nor_2_out, TRES2, d_latch_5_q);
  nor nor_3 (nor_3_out, TRES2, d_latch_7_q);
  nor nor_4 (nor_4_out, TRES2, d_latch_9_q);
  D_Latch d_latch_2 (.NOT_Q(d_latch_2_not_q), .D(nor_1_out), .EN(PHI2));  // open: Q
  D_Latch d_latch_3 (.Q(d_latch_3_q), .D(multiplexer_1_out), .EN(PHI1));  // open: NOT_Q
  D_Latch d_latch_4 (.NOT_Q(d_latch_4_not_q), .D(nor_2_out), .EN(PHI2));  // open: Q
  D_Latch d_latch_5 (.Q(d_latch_5_q), .D(multiplexer_2_out), .EN(PHI1));  // open: NOT_Q
  D_Latch d_latch_6 (.NOT_Q(d_latch_6_not_q), .D(nor_3_out), .EN(PHI2));  // open: Q
  D_Latch d_latch_7 (.Q(d_latch_7_q), .D(multiplexer_3_out), .EN(PHI1));  // open: NOT_Q
  D_Latch d_latch_8 (.NOT_Q(d_latch_8_not_q), .D(nor_4_out), .EN(PHI2));  // open: Q
  D_Latch d_latch_9 (.Q(d_latch_9_q), .D(multiplexer_4_out), .EN(PHI1));  // open: NOT_Q
  not not_1 (L_T2_37fe4d42, nor_1_out);
  not not_2 (L_T3_3fe619b3, nor_2_out);
  not not_3 (L_T4_d9b6e407, nor_3_out);
  not not_4 (L_T5_89b31bc6, nor_4_out);
  not not_5 (not_5_out, undriven);

  // Notes on the sheet:
  //   To test the shift register you must disconnect PHI1 and instead connect PHI2 via an inverter:
  //   PHI2
  //   PHI2
  //   PHI1
endmodule

module ALU_SETUP (
  input  PHI1,
  input  PHI2,
  input  BRFW,
  input  L_READY_a37d69a3,
  input  BRK6E,
  input  STKOP,
  input  D26,
  input  D27,
  input  D29,
  input  D30,
  input  D31,
  input  D32,
  input  D33,
  input  D34,
  input  D35,
  input  D36,
  input  D37,
  input  D38,
  input  D39,
  input  D40,
  input  D41,
  input  D42,
  input  D43,
  input  D44,
  input  D45,
  input  D47,
  input  D48,
  input  D49,
  input  D50,
  input  D51,
  input  D52,
  input  D53,
  input  D54,
  input  D56,
  input  D69,
  input  D70,
  input  D75,
  input  D76,
  input  D84,
  input  D85,
  input  D86,
  input  D87,
  input  D88,
  input  D89,
  input  T0,
  input  T1,
  input  T5,
  input  T6,
  input  PGX,
  input  BR3,
  input  L_D_OUT_7d61c6e7,
  input  L_C_OUT_f91ece9c,
  output NDB_ADD_ee0a1870,
  output DB_ADD_48d85b7e,
  output L_0_ADD_81d17e61,
  output SB_ADD_0eab26ac,
  output ADL_ADD_e28b8a30,
  output AND,
  output ANDS,
  output EORS,
  output ORS,
  output L_ACIN_e173f520,
  output SRS,
  output SUMS,
  output L_DAA_82b80d94,
  output ADD_SB7_a8f4b77a,
  output ADD_SB06_a3738230,
  output ADD_ADL_3fac4345,
  output L_DSA_ea96e89b,
  output INC_SB,
  output SR
);

  wire and_1_out, buffer_1_out, buffer_2_out, buffer_3_out, buffer_4_out, buffer_5_out, d_latch_1_q,
       d_latch_2_q, d_latch_3_q, d_latch_4_q, d_latch_5_not_q, d_latch_6_q, d_latch_7_q, d_latch_8_q,
       d_latch_9_q, d_latch_10_not_q, d_latch_11_not_q, d_latch_12_not_q, d_latch_13_not_q, d_latch_14_not_q,
       d_latch_15_not_q, d_latch_16_not_q, d_latch_17_not_q, d_latch_18_not_q, d_latch_19_not_q,
       d_latch_20_not_q, d_latch_21_not_q, d_latch_22_not_q, d_latch_23_not_q, d_latch_24_not_q,
       d_latch_25_not_q, d_latch_26_not_q, d_latch_27_not_q, d_latch_28_not_q, d_latch_29_not_q,
       d_latch_30_not_q, d_latch_31_not_q, d_latch_32_not_q, d_latch_33_not_q, L_1_28cbbb7d_out,
       L_3_39a566ac_out, L_4_558283f2_out, L_8_05eb4f56_out, L_11_aa2e7fa3_out, L_14_4f483598_out,
       L_15_5dad5732_out, L_17_0f5278c7_out, L_19_e094c090_out, L_20_adeacd1b_out, L_22_f545d19e_out,
       L_24_b6efc2f4_out, L_25_f5ad6aee_out, L_27_6492a6f4_out, L_29_1d3a3eb3_out, L_31_e958c8e2_out,
       L_32_7de83e69_out, L_33_cae225fb_out, L_34_97db28cb_out, L_35_8b2262aa_out, L_37_acfb42d2_out,
       L_40_1e6b68e0_out, L_41_b24af141_out, L_42_ae8bf3e0_out, L_44_bb416d4b_out, L_45_e516ed8c_out,
       L_48_330a6f3f_out, L_56_35bf93dd_out, L_61_ef440803_out, L_73_3c19a6e4_out, multiplexer_1_out,
       nor_1_out, nor_2_out, nor_3_out, nor_4_out, nor_5_out, not_1_out, not_3_out, not_4_out, not_5_out,
       not_8_out, not_9_out, not_10_out, not_11_out, not_12_out, not_13_out, not_14_out, not_15_out,
       not_16_out, not_17_out;

  and L_17_0f5278c7 (L_17_0f5278c7_out, D33, not_1_out);
  not not_1 (not_1_out, D34);
  and and_1 (and_1_out, T5, D44);
  or L_31_e958c8e2 (L_31_e958c8e2_out, D52, D53);
  nor L_1_28cbbb7d (L_1_28cbbb7d_out, D69, D70);
  not not_2 (AND, L_1_28cbbb7d_out);
  and L_3_39a566ac (L_3_39a566ac_out, D76, T5);
  not not_3 (not_3_out, D27);
  nor L_15_5dad5732 (L_15_5dad5732_out, D32, L_READY_a37d69a3);
  not not_4 (not_4_out, L_15_5dad5732_out);
  not not_5 (not_5_out, BR3);
  nor L_4_558283f2 (L_4_558283f2_out, D75, L_3_39a566ac_out);
  not not_6 (SR, L_4_558283f2_out);
  nor L_42_ae8bf3e0 (L_42_ae8bf3e0_out, D84, D85, D86, D87, D88, D89, D26);
  nor L_19_e094c090 (L_19_e094c090_out, L_17_0f5278c7_out, D35, D36, D37, D38, D39, L_READY_a37d69a3);
  nor L_20_adeacd1b (L_20_adeacd1b_out, D39, D40, D41, D42, D43, and_1_out);
  not not_7 (INC_SB, L_20_adeacd1b_out);
  nor L_29_1d3a3eb3 (L_29_1d3a3eb3_out, not_5_out, BRFW);
  nor L_34_97db28cb (L_34_97db28cb_out, T0, T5);
  not not_8 (not_8_out, D47);
  nor L_27_6492a6f4 (L_27_6492a6f4_out, D49, D50, L_29_1d3a3eb3_out);
  not not_9 (not_9_out, L_27_6492a6f4_out);
  nor L_35_8b2262aa (L_35_8b2262aa_out, L_C_OUT_f91ece9c, L_34_97db28cb_out);
  nor L_14_4f483598 (L_14_4f483598_out, STKOP, D30, D31, D45, D48, INC_SB, D47, BRK6E, L_READY_a37d69a3);
  nor L_24_b6efc2f4 (L_24_b6efc2f4_out, L_19_e094c090_out, not_8_out);
  nor L_32_7de83e69 (L_32_7de83e69_out, L_35_8b2262aa_out, L_31_e958c8e2_out);
  not not_10 (not_10_out, D54);
  nand L_33_cae225fb (L_33_cae225fb_out, L_32_7de83e69_out, not_10_out);
  nand L_40_1e6b68e0 (L_40_1e6b68e0_out, D52, L_D_OUT_7d61c6e7);
  or L_44_bb416d4b (L_44_bb416d4b_out, not_9_out, D56, D51);
  D_Latch d_latch_1 (.Q(d_latch_1_q), .D(L_24_b6efc2f4_out), .EN(PHI2));  // open: NOT_Q
  D_Latch d_latch_2 (.Q(d_latch_2_q), .D(INC_SB), .EN(PHI2));  // open: NOT_Q
  D_Latch d_latch_3 (.Q(d_latch_3_q), .D(not_9_out), .EN(PHI2));  // open: NOT_Q
  D_Latch d_latch_4 (.Q(d_latch_4_q), .D(L_33_cae225fb_out), .EN(PHI2));  // open: NOT_Q
  D_Latch d_latch_5 (.NOT_Q(d_latch_5_not_q), .D(SR), .EN(PHI2));  // open: Q
  not not_11 (not_11_out, SR);
  D_Latch d_latch_6 (.Q(d_latch_6_q), .D(L_READY_a37d69a3), .EN(PHI1));  // open: NOT_Q
  nor L_41_b24af141 (L_41_b24af141_out, L_42_ae8bf3e0_out, PGX);
  nor L_56_35bf93dd (L_56_35bf93dd_out, L_40_1e6b68e0_out, D51);
  nand L_37_acfb42d2 (L_37_acfb42d2_out, D51, L_D_OUT_7d61c6e7);
  not not_12 (not_12_out, L_READY_a37d69a3);
  nor L_8_05eb4f56 (L_8_05eb4f56_out, not_11_out, d_latch_6_q);
  not not_13 (not_13_out, L_C_OUT_f91ece9c);
  not not_14 (not_14_out, L_41_b24af141_out);
  not not_15 (not_15_out, L_56_35bf93dd_out);
  nand L_45_e516ed8c (L_45_e516ed8c_out, L_44_bb416d4b_out, not_12_out);
  nor L_25_f5ad6aee (L_25_f5ad6aee_out, d_latch_1_q, d_latch_2_q, d_latch_3_q, d_latch_4_q);
  D_Latch d_latch_7 (.Q(d_latch_7_q), .D(d_latch_5_not_q), .EN(PHI1));  // open: NOT_Q
  D_Latch d_latch_8 (.Q(d_latch_8_q), .D(L_8_05eb4f56_out), .EN(PHI2));  // open: NOT_Q
  D_Latch d_latch_9 (.Q(d_latch_9_q), .D(d_latch_11_not_q), .EN(PHI2));  // open: NOT_Q
  D_Latch d_latch_10 (.NOT_Q(d_latch_10_not_q), .D(not_13_out), .EN(PHI2));  // open: Q
  not not_16 (not_16_out, multiplexer_1_out);
  Multiplexer multiplexer_1 (.in0(d_latch_9_q), .in1(d_latch_10_not_q), .out(multiplexer_1_out), .sel(d_latch_8_q));
  nand L_48_330a6f3f (L_48_330a6f3f_out, L_45_e516ed8c_out, L_19_e094c090_out);
  nor L_73_3c19a6e4 (L_73_3c19a6e4_out, AND, D29, not_4_out, SR);
  nor L_22_f545d19e (L_22_f545d19e_out, T6, PGX);
  nor L_11_aa2e7fa3 (L_11_aa2e7fa3_out, not_3_out, d_latch_7_q, d_latch_11_not_q);
  D_Latch d_latch_11 (.NOT_Q(d_latch_11_not_q), .D(not_16_out), .EN(PHI1));  // open: Q
  not not_17 (not_17_out, L_14_4f483598_out);
  nor L_61_ef440803 (L_61_ef440803_out, L_11_aa2e7fa3_out, L_22_f545d19e_out);
  D_Latch d_latch_12 (.NOT_Q(d_latch_12_not_q), .D(L_45_e516ed8c_out), .EN(PHI2));  // open: Q
  D_Latch d_latch_13 (.NOT_Q(d_latch_13_not_q), .D(L_48_330a6f3f_out), .EN(PHI2));  // open: Q
  D_Latch d_latch_14 (.NOT_Q(d_latch_14_not_q), .D(L_14_4f483598_out), .EN(PHI2));  // open: Q
  D_Latch d_latch_15 (.NOT_Q(d_latch_15_not_q), .D(not_17_out), .EN(PHI2));  // open: Q
  D_Latch d_latch_16 (.NOT_Q(d_latch_16_not_q), .D(L_19_e094c090_out), .EN(PHI2));  // open: Q
  D_Latch d_latch_17 (.NOT_Q(d_latch_17_not_q), .D(AND), .EN(PHI2));  // open: Q
  D_Latch d_latch_18 (.NOT_Q(d_latch_18_not_q), .D(D29), .EN(PHI2));  // open: Q
  D_Latch d_latch_19 (.NOT_Q(d_latch_19_not_q), .D(not_4_out), .EN(PHI2));  // open: Q
  D_Latch d_latch_20 (.NOT_Q(d_latch_20_not_q), .D(SR), .EN(PHI2));  // open: Q
  D_Latch d_latch_21 (.NOT_Q(d_latch_21_not_q), .D(L_73_3c19a6e4_out), .EN(PHI2));  // open: Q
  D_Latch d_latch_22 (.NOT_Q(d_latch_22_not_q), .D(not_15_out), .EN(PHI2));  // open: Q
  D_Latch d_latch_23 (.NOT_Q(d_latch_23_not_q), .D(L_61_ef440803_out), .EN(PHI2));  // open: Q
  D_Latch d_latch_24 (.NOT_Q(d_latch_24_not_q), .D(L_22_f545d19e_out), .EN(PHI2));  // open: Q
  D_Latch d_latch_25 (.NOT_Q(d_latch_25_not_q), .D(not_14_out), .EN(PHI2));  // open: Q
  D_Latch d_latch_26 (.NOT_Q(d_latch_26_not_q), .D(L_37_acfb42d2_out), .EN(PHI2));  // open: Q
  nor nor_1 (nor_1_out, PHI2, d_latch_12_not_q);
  nor nor_2 (nor_2_out, PHI2, d_latch_13_not_q);
  nor nor_3 (nor_3_out, PHI2, d_latch_14_not_q);
  nor nor_4 (nor_4_out, PHI2, d_latch_15_not_q);
  nor nor_5 (nor_5_out, PHI2, d_latch_16_not_q);
  D_Latch d_latch_27 (.NOT_Q(d_latch_27_not_q), .D(d_latch_17_not_q), .EN(PHI1));  // open: Q
  D_Latch d_latch_28 (.NOT_Q(d_latch_28_not_q), .D(d_latch_18_not_q), .EN(PHI1));  // open: Q
  D_Latch d_latch_29 (.NOT_Q(d_latch_29_not_q), .D(d_latch_19_not_q), .EN(PHI1));  // open: Q
  D_Latch d_latch_30 (.NOT_Q(d_latch_30_not_q), .D(L_25_f5ad6aee_out), .EN(PHI1));  // open: Q
  D_Latch d_latch_31 (.NOT_Q(d_latch_31_not_q), .D(d_latch_20_not_q), .EN(PHI1));  // open: Q
  D_Latch d_latch_32 (.NOT_Q(d_latch_32_not_q), .D(d_latch_21_not_q), .EN(PHI1));  // open: Q
  D_Latch d_latch_33 (.NOT_Q(d_latch_33_not_q), .D(d_latch_22_not_q), .EN(PHI1));  // open: Q
  D_Latch d_latch_34 (.NOT_Q(L_DSA_ea96e89b), .D(d_latch_26_not_q), .EN(PHI1));  // open: Q
  nor nor_6 (NDB_ADD_ee0a1870, PHI2, buffer_1_out);
  buf buffer_1 (buffer_1_out, nor_1_out);
  nor nor_7 (DB_ADD_48d85b7e, PHI2, buffer_2_out);
  buf buffer_2 (buffer_2_out, nor_2_out);
  nor nor_8 (L_0_ADD_81d17e61, PHI2, buffer_3_out);
  buf buffer_3 (buffer_3_out, nor_3_out);
  nor nor_9 (SB_ADD_0eab26ac, PHI2, buffer_4_out);
  buf buffer_4 (buffer_4_out, nor_4_out);
  nor nor_10 (ADL_ADD_e28b8a30, PHI2, buffer_5_out);
  buf buffer_5 (buffer_5_out, nor_5_out);
  buf buffer_6 (ANDS, d_latch_27_not_q);
  buf buffer_7 (EORS, d_latch_28_not_q);
  buf buffer_8 (ORS, d_latch_29_not_q);
  not not_18 (L_ACIN_e173f520, d_latch_30_not_q);
  buf buffer_9 (SRS, d_latch_31_not_q);
  buf buffer_10 (SUMS, d_latch_32_not_q);
  buf buffer_11 (L_DAA_82b80d94, d_latch_33_not_q);
  buf buffer_12 (ADD_SB7_a8f4b77a, d_latch_23_not_q);
  buf buffer_13 (ADD_SB06_a3738230, d_latch_24_not_q);
  buf buffer_14 (ADD_ADL_3fac4345, d_latch_25_not_q);

  // Other names for the same wires on the sheet: JSR_5_a4d207ab = D56; L_ready_9a3f8f92 = L_READY_a37d69a3;
  //   RTI_5_727c5a3b = D26; RTS_5_475d8b78 = D84; SBC0 = D51

  // Notes on the sheet:
  //   ROR
  //   EOR
  //   18
  //   STK2
  //   JSR2
  //   RET
  //   JSR2
  //   2
  //   6
  //   16
  //   OR
  //   5
  //   NOADL
  //   21
  //   23
  //   28
  //   #ADL/ADD
  //   BRX
  //   30
  //   SB/ADD
  //   CSET
  //   25,1
  //   25,2
  //   25,3
  //   25,4
  //   PGX
  //   10
  //   9
  //   8
  //   62
  //   39
  //   43
  //   /ACIN
  //   11
  //   13,3 13,1
  //   13,2
  //   7
  //   #NDB/ADD
  //   12
  //   51
  //   #ADL/ADD
  //   66
  //   67
  //   68
  //   69
  //   70
  //   64
  //   #ADD/SB7
  //   58
  //   #ADD/SB06
  //   59
  //   60
  //   38
  //   46
  //   47
  //   49
  //   50
  //   53
  //   55
  //   /ACIN
  //   72
  //   57
  //   54
  //   71
  //   56
  //   63
  //   65
endmodule

module BRANCH_LOGIC (
  input  L_IR5_9e15d54c,
  input  D121,
  input  D126,
  input  L_C_OUT_f91ece9c,
  input  L_V_OUT_959779aa,
  input  L_N_OUT_10df9d15,
  input  L_Z_OUT_2813b2ba,
  input  PHI1,
  input  PHI2,
  input  DB7,
  input  BR2,
  output L_BRTAKEN_ace66327,
  output BRFW
);

  wire d_latch_1_q, d_latch_2_q, d_latch_3_not_q, multiplexer_1_out, nor_1_out, nor_2_out, nor_3_out,
       nor_4_out, nor_5_out, not_1_out, not_2_out, not_3_out, not_4_out, not_5_out, not_6_out;

  not not_1 (not_1_out, D121);
  not not_2 (not_2_out, D126);
  not not_3 (not_3_out, D126);
  not not_4 (not_4_out, D121);
  not not_5 (not_5_out, DB7);
  D_Latch d_latch_1 (.Q(d_latch_1_q), .D(BR2), .EN(PHI2));  // open: NOT_Q
  D_Latch d_latch_2 (.Q(d_latch_2_q), .D(d_latch_3_not_q), .EN(PHI2));  // open: NOT_Q
  nor nor_1 (nor_1_out, L_C_OUT_f91ece9c, D126, not_1_out);
  nor nor_2 (nor_2_out, L_V_OUT_959779aa, D121, not_2_out);
  nor nor_3 (nor_3_out, L_N_OUT_10df9d15, not_3_out, not_4_out);
  nor nor_4 (nor_4_out, D126, D121, L_Z_OUT_2813b2ba);
  nor nor_5 (nor_5_out, nor_1_out, nor_2_out, nor_3_out, nor_4_out);
  Multiplexer multiplexer_1 (.in0(d_latch_2_q), .in1(not_5_out), .out(multiplexer_1_out), .sel(d_latch_1_q));
  xor xor_1 (L_BRTAKEN_ace66327, L_IR5_9e15d54c, nor_5_out);
  not not_6 (not_6_out, multiplexer_1_out);
  D_Latch d_latch_3 (.NOT_Q(d_latch_3_not_q), .D(not_6_out), .EN(PHI1));  // open: Q
  not not_7 (BRFW, d_latch_3_not_q);

  // Notes on the sheet:
  //   /IR7
endmodule

// PROGRAM COUNTER SETUP
module PC_SETUP (
  input  PHI1,
  input  PHI2,
  input  D56,
  input  D77,
  input  D78,
  input  D83,
  input  D84,
  input  D94,
  input  D95,
  input  D96,
  input  D129,
  input  L_READY_a37d69a3,
  input  BR3,
  input  BR2,
  input  T0,
  input  T1,
  input  BR0,
  output PCL_DB_4172714e,
  output PCH_DB_a81fefa0,
  output PC_DB_a835deaa,
  output PCL_ADL_ee043dbc,
  output PCH_ADH_ead93594,
  output PCL_PCL_4f350f4d,
  output ADL_PCL_9a95c372,
  output L_ADL_PCL_a2520980,
  output DL_PCH_0dc37cb4,
  output ADH_PCH_61520abf,
  output PCH_PCH_807b9fbd,
  output L_PCH_PCH_e0d9e687
);

  wire buffer_5_out, buffer_6_out, buffer_7_out, buffer_8_out, d_latch_1_q, d_latch_2_q, d_latch_3_not_q,
       d_latch_4_not_q, d_latch_5_not_q, d_latch_6_not_q, d_latch_7_not_q, d_latch_8_not_q, d_latch_9_not_q,
       d_latch_10_not_q, d_latch_11_not_q, L_1_28cbbb7d_out, L_2_143403ae_out, L_3_39a566ac_out,
       L_4_558283f2_out, L_9_0082242d_out, L_11_aa2e7fa3_out, L_12_85a3418f_out, L_14_4f483598_out,
       L_16_c7396848_out, L_17_0f5278c7_out, nor_2_out, nor_3_out, nor_4_out, nor_5_out, nor_6_out,
       not_1_out, not_2_out, not_3_out, not_5_out;

  nor L_3_39a566ac (L_3_39a566ac_out, D94, D95, D96);
  nor L_1_28cbbb7d (L_1_28cbbb7d_out, D77, D78);
  nor L_2_143403ae (L_2_143403ae_out, D83, D129);
  D_Latch d_latch_1 (.Q(d_latch_1_q), .D(L_1_28cbbb7d_out), .EN(PHI2));  // open: NOT_Q
  D_Latch d_latch_2 (.Q(d_latch_2_q), .D(L_READY_a37d69a3), .EN(PHI1));  // open: NOT_Q
  nor L_4_558283f2 (L_4_558283f2_out, d_latch_1_q, L_READY_a37d69a3);
  nor L_16_c7396848 (L_16_c7396848_out, L_3_39a566ac_out, d_latch_2_q);
  not not_1 (not_1_out, d_latch_2_q);
  not not_2 (not_2_out, T0);
  nor L_14_4f483598 (L_14_4f483598_out, L_16_c7396848_out, not_2_out);
  and L_9_0082242d (L_9_0082242d_out, not_1_out, BR3);
  nor L_15_5dad5732 (DL_PCH_0dc37cb4, not_2_out, L_3_39a566ac_out);
  D_Latch d_latch_3 (.NOT_Q(d_latch_3_not_q), .D(L_4_558283f2_out), .EN(PHI1));  // open: Q
  not not_3 (not_3_out, L_12_85a3418f_out);
  nand L_6_5b7e39b9 (PC_DB_a835deaa, d_latch_3_not_q, L_1_28cbbb7d_out);
  nor L_12_85a3418f (L_12_85a3418f_out, T1, BR2);
  nor nor_1 (L_ADL_PCL_a2520980, not_3_out, D84, T0, L_9_0082242d_out);
  nor nor_2 (nor_2_out, D84, L_2_143403ae_out, T0, T1, BR2, BR3);
  nor L_11_aa2e7fa3 (L_11_aa2e7fa3_out, L_12_85a3418f_out, DL_PCH_0dc37cb4, BR0);
  not not_4 (L_PCH_PCH_e0d9e687, nor_2_out);
  nor L_17_0f5278c7 (L_17_0f5278c7_out, L_11_aa2e7fa3_out, BR3);
  not not_5 (not_5_out, L_ADL_PCL_a2520980);
  D_Latch d_latch_4 (.NOT_Q(d_latch_4_not_q), .D(d_latch_3_not_q), .EN(PHI2));  // open: Q
  D_Latch d_latch_5 (.NOT_Q(d_latch_5_not_q), .D(L_1_28cbbb7d_out), .EN(PHI2));  // open: Q
  D_Latch d_latch_6 (.NOT_Q(d_latch_6_not_q), .D(L_12_85a3418f_out), .EN(PHI2));  // open: Q
  D_Latch d_latch_7 (.NOT_Q(d_latch_7_not_q), .D(L_17_0f5278c7_out), .EN(PHI2));  // open: Q
  D_Latch d_latch_8 (.NOT_Q(d_latch_8_not_q), .D(not_5_out), .EN(PHI2));  // open: Q
  D_Latch d_latch_9 (.NOT_Q(d_latch_9_not_q), .D(L_ADL_PCL_a2520980), .EN(PHI2));  // open: Q
  D_Latch d_latch_10 (.NOT_Q(d_latch_10_not_q), .D(nor_2_out), .EN(PHI2));  // open: Q
  D_Latch d_latch_11 (.NOT_Q(d_latch_11_not_q), .D(L_PCH_PCH_e0d9e687), .EN(PHI2));  // open: Q
  buf buffer_1 (PCL_DB_4172714e, d_latch_4_not_q);
  buf buffer_2 (PCH_DB_a81fefa0, d_latch_5_not_q);
  buf buffer_3 (PCL_ADL_ee043dbc, d_latch_6_not_q);
  buf buffer_4 (PCH_ADH_ead93594, d_latch_7_not_q);
  nor nor_3 (nor_3_out, PHI2, d_latch_8_not_q);
  buf buffer_5 (buffer_5_out, nor_3_out);
  nor nor_4 (nor_4_out, PHI2, d_latch_9_not_q);
  buf buffer_6 (buffer_6_out, nor_4_out);
  nor nor_5 (nor_5_out, PHI2, d_latch_10_not_q);
  buf buffer_7 (buffer_7_out, nor_5_out);
  nor nor_6 (nor_6_out, PHI2, d_latch_11_not_q);
  buf buffer_8 (buffer_8_out, nor_6_out);
  nor nor_7 (PCL_PCL_4f350f4d, PHI2, buffer_5_out);
  nor nor_8 (ADL_PCL_9a95c372, PHI2, buffer_6_out);
  nor nor_9 (ADH_PCH_61520abf, PHI2, buffer_7_out);
  nor nor_10 (PCH_PCH_807b9fbd, PHI2, buffer_8_out);

  // Other names for the same wires on the sheet: RTS_5_475d8b78 = D84

  // Notes on the sheet:
  //   JRS5
  //   Push/pull
  //   JB
  //   4
  //   16
  //   #PCH/DB
  //   ABS/2
  //   16
  //   3
  //   5
  //   18
  //   DL/PCH
  //   #PCL/DB
  //   PC/DB
  //   DL/PCH
  //   #PCL/ADL
  //   #ADL/PCL
  //   #ADH/PCH
  //   7
  //   8
endmodule

module DISPATCH (
  input  PHI1,
  input  PHI2,
  input  BRK6E,
  input  BR2,
  input  RESP,
  input  ACR,
  input  DORES,
  input  PC_DB_a835deaa,
  input  D91,
  input  D92,
  input  BR3,
  input  D96,
  input  D97,
  input  D98,
  input  D100,
  input  D101,
  input  D102,
  input  D103,
  input  D104,
  input  D105,
  input  D106,
  input  D107,
  input  D111,
  input  D122,
  input  D123,
  input  D124,
  input  D125,
  input  RDY,
  input  B_OUT,
  input  BRFW,
  input  L_BRTAKEN_ace66327,
  input  L_TWOCYCLE_54b4f369,
  input  L_ADL_PCL_a2520980,
  input  L_IMPLED_6d196eb4,
  output ACRL2,
  output T5,
  output T6,
  output TRES2,
  output TRESX,
  output STOR,
  output ENDX_Debug,
  output ENDS_Debug,
  output L_0_IR_c32b8001,
  output FETCH,
  output L_READY_a37d69a3,
  output RD,
  output R_W_47630a0a,
  output WR,
  output T1,
  output TRES1,
  output L_T0_5a901129,
  output T0,
  output L_T1X_624de7e6,
  output L_1_PC_1c371e3f
);

  wire and_1_out, d_latch_1_not_q, d_latch_2_not_q, d_latch_4_q, d_latch_5_q, d_latch_6_q, d_latch_7_q,
       d_latch_8_q, d_latch_9_not_q, d_latch_11_q, d_latch_12_q, d_latch_13_q, d_latch_14_q, d_latch_15_q,
       d_latch_16_not_q, d_latch_17_not_q, d_latch_18_not_q, d_latch_19_not_q, d_latch_20_q, d_latch_21_q,
       d_latch_22_q, d_latch_24_q, d_latch_25_q, d_latch_26_q, d_latch_27_q, d_latch_28_q, d_latch_29_q,
       d_latch_31_not_q, d_latch_33_not_q, L_1_28cbbb7d_out, L_2_143403ae_out, L_5_9518e519_out,
       L_6_5b7e39b9_out, L_9_0082242d_out, L_11_aa2e7fa3_out, L_13_587da886_out, L_15_5dad5732_out,
       L_17_0f5278c7_out, L_21_ada5c31c_out, L_22_f545d19e_out, L_24_b6efc2f4_out, L_25_f5ad6aee_out,
       L_26_ffeee2da_out, L_30_3bf8f3d0_out, L_31_e958c8e2_out, L_33_cae225fb_out, L_37_acfb42d2_out,
       L_38_43aa51c3_out, L_39_c97a3f22_out, L_43_fdaf143b_out, L_47_7c60183d_out, L_50_6b408103_out,
       L_53_d08b6e35_out, L_54_01afe50f_out, L_56_35bf93dd_out, L_65_6a42b4dc_out, L_73_3c19a6e4_out,
       L_78_8a0d457e_out, L_MemOP_bf72a9c8, L_SHIFT_2aa3590c, multiplexer_1_out, nor_1_out, nor_2_out,
       nor_3_out, nor_4_out, not_1_out, not_2_out, not_3_out, not_4_out, not_5_out, not_6_out, not_7_out,
       not_8_out, not_9_out, not_10_out, not_11_out, NotReadyPhi1, or_1_out, xor_1_out;

  nor L_1_28cbbb7d (L_1_28cbbb7d_out, D91, D92);
  not not_1 (not_1_out, D97);
  nor L_13_587da886 (L_13_587da886_out, BR2, BR3);
  not not_2 (not_2_out, NotReadyPhi1);
  nor L_33_cae225fb (L_33_cae225fb_out, D100, D101, D102, D103, D104, D105);
  nor L_32_7de83e69 (L_SHIFT_2aa3590c, D106, D107);
  nor L_51_79fb832a (L_MemOP_bf72a9c8, D111, D125);
  not not_3 (not_3_out, L_13_587da886_out);
  not not_4 (not_4_out, L_IMPLED_6d196eb4);
  not not_5 (not_5_out, ACR);
  and L_73_3c19a6e4 (L_73_3c19a6e4_out, not_5_out, not_2_out);
  nor L_78_8a0d457e (L_78_8a0d457e_out, not_2_out, ACRL2);
  not not_6 (not_6_out, L_33_cae225fb_out);
  and L_9_0082242d (L_9_0082242d_out, L_BRTAKEN_ace66327, BR2);
  not not_7 (not_7_out, BR3);
  and L_17_0f5278c7 (L_17_0f5278c7_out, L_BRTAKEN_ace66327, BR2);
  nor L_15_5dad5732 (L_15_5dad5732_out, L_ADL_PCL_a2520980, not_3_out);
  nor nor_1 (nor_1_out, L_73_3c19a6e4_out, L_78_8a0d457e_out);
  nor L_37_acfb42d2 (L_37_acfb42d2_out, T5, T6, D100, D98, PC_DB_a835deaa, STOR);
  nor nor_2 (nor_2_out, T0, L_9_0082242d_out);
  Multiplexer multiplexer_1 (.in0(nor_2_out), .in1(not_8_out), .out(multiplexer_1_out), .sel(L_READY_a37d69a3));
  not not_8 (not_8_out, T1);
  nor L_21_ada5c31c (L_21_ada5c31c_out, not_7_out, NotReadyPhi1);
  D_Latch d_latch_1 (.NOT_Q(d_latch_1_not_q), .D(L_READY_a37d69a3), .EN(PHI1));  // open: Q
  nor nor_3 (nor_3_out, L_17_0f5278c7_out, L_15_5dad5732_out);
  not not_9 (not_9_out, L_SHIFT_2aa3590c);
  not not_10 (not_10_out, L_READY_a37d69a3);
  D_Latch d_latch_2 (.NOT_Q(d_latch_2_not_q), .D(nor_1_out), .EN(PHI1));  // open: Q
  D_Latch d_latch_3 (.NOT_Q(ACRL2), .D(d_latch_2_not_q), .EN(PHI2));  // open: Q
  D_Latch d_latch_4 (.Q(d_latch_4_q), .D(L_1_28cbbb7d_out), .EN(PHI2));  // open: NOT_Q
  nor L_11_aa2e7fa3 (L_11_aa2e7fa3_out, D96, not_9_out, L_MemOP_bf72a9c8);
  D_Latch d_latch_5 (.Q(d_latch_5_q), .D(L_37_acfb42d2_out), .EN(PHI2));  // open: NOT_Q
  D_Latch d_latch_6 (.Q(d_latch_6_q), .D(multiplexer_1_out), .EN(PHI2));  // open: NOT_Q
  D_Latch d_latch_7 (.Q(d_latch_7_q), .D(RESP), .EN(PHI2));  // open: NOT_Q
  D_Latch d_latch_8 (.Q(d_latch_8_q), .D(not_10_out), .EN(PHI1));  // open: NOT_Q
  D_Latch d_latch_9 (.NOT_Q(d_latch_9_not_q), .D(L_21_ada5c31c_out), .EN(PHI2));  // open: Q
  xor xor_1 (xor_1_out, BRFW, ACR);
  D_Latch d_latch_10 (.NOT_Q(NotReadyPhi1), .D(d_latch_1_not_q), .EN(PHI2));  // open: Q
  D_Latch d_latch_11 (.Q(d_latch_11_q), .D(TRES1), .EN(PHI1));  // open: NOT_Q
  D_Latch d_latch_12 (.Q(d_latch_12_q), .D(L_TWOCYCLE_54b4f369), .EN(PHI1));  // open: NOT_Q
  D_Latch d_latch_13 (.Q(d_latch_13_q), .D(TRESX), .EN(PHI1));  // open: NOT_Q
  D_Latch d_latch_14 (.Q(d_latch_14_q), .D(nor_3_out), .EN(PHI2));  // open: NOT_Q
  nand L_38_43aa51c3 (L_38_43aa51c3_out, L_SHIFT_2aa3590c, not_1_out);
  nor L_12_85a3418f (ENDX_Debug, L_11_aa2e7fa3_out, T6, not_6_out, BR3);
  nor L_8_05eb4f56 (ENDS_Debug, d_latch_6_q, d_latch_7_q);
  nor L_24_b6efc2f4 (L_24_b6efc2f4_out, d_latch_9_not_q, xor_1_out);
  and and_1 (and_1_out, d_latch_12_q, d_latch_13_q);
  nor L_43_fdaf143b (L_43_fdaf143b_out, L_SHIFT_2aa3590c, L_MemOP_bf72a9c8, L_READY_a37d69a3);
  not not_11 (not_11_out, L_READY_a37d69a3);
  nor L_56_35bf93dd (L_56_35bf93dd_out, d_latch_11_q, and_1_out);
  nor L_54_01afe50f (L_54_01afe50f_out, d_latch_24_q, d_latch_25_q);
  D_Latch d_latch_15 (.Q(d_latch_15_q), .D(L_43_fdaf143b_out), .EN(PHI2));  // open: NOT_Q
  nand L_47_7c60183d (L_47_7c60183d_out, T5, not_11_out);
  nor L_2_143403ae (L_2_143403ae_out, nor_1_out, d_latch_4_q, L_READY_a37d69a3, L_38_43aa51c3_out);
  nor L_5_9518e519 (L_5_9518e519_out, RESP, ENDS_Debug, L_6_5b7e39b9_out);
  nor L_39_c97a3f22 (L_39_c97a3f22_out, RDY, d_latch_20_q);
  nor L_40_1e6b68e0 (WR, L_READY_a37d69a3, d_latch_5_q, DORES);
  nor L_26_ffeee2da (L_26_ffeee2da_out, d_latch_8_q, RESP, d_latch_22_q);
  nor L_25_f5ad6aee (L_25_f5ad6aee_out, d_latch_21_q, L_24_b6efc2f4_out);
  nor L_31_e958c8e2 (L_31_e958c8e2_out, L_25_f5ad6aee_out, L_READY_a37d69a3);
  nor L_30_3bf8f3d0 (L_30_3bf8f3d0_out, L_31_e958c8e2_out, ENDS_Debug);
  nor L_57_0f0af090 (L_T0_5a901129, L_56_35bf93dd_out, L_54_01afe50f_out);
  nor L_53_d08b6e35 (L_53_d08b6e35_out, d_latch_24_q, L_READY_a37d69a3);
  nor L_22_f545d19e (L_22_f545d19e_out, L_READY_a37d69a3, d_latch_14_q, not_4_out);
  and L_50_6b408103 (L_50_6b408103_out, d_latch_29_q, L_READY_a37d69a3);
  D_Latch d_latch_16 (.NOT_Q(d_latch_16_not_q), .D(L_47_7c60183d_out), .EN(PHI2));  // open: Q
  D_Latch d_latch_17 (.NOT_Q(d_latch_17_not_q), .D(L_5_9518e519_out), .EN(PHI2));  // open: Q
  D_Latch d_latch_18 (.NOT_Q(d_latch_18_not_q), .D(T1), .EN(PHI2));  // open: Q
  D_Latch d_latch_19 (.NOT_Q(d_latch_19_not_q), .D(L_39_c97a3f22_out), .EN(PHI2));  // open: Q
  D_Latch d_latch_20 (.Q(d_latch_20_q), .D(WR), .EN(PHI1));  // open: NOT_Q
  D_Latch d_latch_21 (.Q(d_latch_21_q), .D(L_26_ffeee2da_out), .EN(PHI2));  // open: NOT_Q
  D_Latch d_latch_22 (.Q(d_latch_22_q), .D(L_25_f5ad6aee_out), .EN(PHI1));  // open: NOT_Q
  D_Latch d_latch_23 (.NOT_Q(T1), .D(L_30_3bf8f3d0_out), .EN(PHI1));  // open: Q
  not not_12 (TRES1, L_30_3bf8f3d0_out);
  D_Latch d_latch_24 (.Q(d_latch_24_q), .D(L_T0_5a901129), .EN(PHI2));  // open: NOT_Q
  D_Latch d_latch_25 (.Q(d_latch_25_q), .NOT_Q(L_T1X_624de7e6), .D(L_53_d08b6e35_out), .EN(PHI1));
  D_Latch d_latch_26 (.Q(d_latch_26_q), .D(B_OUT), .EN(PHI1));  // open: NOT_Q
  D_Latch d_latch_27 (.Q(d_latch_27_q), .D(L_24_b6efc2f4_out), .EN(PHI1));  // open: NOT_Q
  D_Latch d_latch_28 (.Q(d_latch_28_q), .D(L_22_f545d19e_out), .EN(PHI1));  // open: NOT_Q
  nor nor_4 (nor_4_out, L_50_6b408103_out, d_latch_15_q);
  nor L_3_39a566ac (TRESX, L_2_143403ae_out, BRK6E, d_latch_17_not_q);
  nor L_36_34609549 (STOR, L_MemOP_bf72a9c8, not_1_out);
  not not_13 (L_READY_a37d69a3, d_latch_19_not_q);
  D_Latch d_latch_29 (.Q(d_latch_29_q), .D(T5), .EN(PHI2));  // open: NOT_Q
  D_Latch d_latch_30 (.NOT_Q(T5), .D(nor_4_out), .EN(PHI1));  // open: Q
  D_Latch d_latch_31 (.NOT_Q(d_latch_31_not_q), .D(d_latch_16_not_q), .EN(PHI1));  // open: Q
  not not_14 (T6, d_latch_31_not_q);
  D_Latch d_latch_32 (.NOT_Q(TRES2), .D(TRESX), .EN(PHI1));  // open: Q
  nor L_6_5b7e39b9 (L_6_5b7e39b9_out, L_READY_a37d69a3, ENDX_Debug);
  nor L_60_8c46ae22 (FETCH, d_latch_18_not_q, L_READY_a37d69a3);
  D_Latch d_latch_33 (.NOT_Q(d_latch_33_not_q), .D(WR), .EN(PHI1));  // open: Q
  not not_15 (T0, L_T0_5a901129);
  or or_1 (or_1_out, d_latch_27_q, d_latch_28_q);
  nand L_61_ef440803 (L_0_IR_c32b8001, B_OUT, FETCH);
  nor L_65_6a42b4dc (L_65_6a42b4dc_out, PHI1, d_latch_33_not_q);
  not not_16 (RD, L_65_6a42b4dc_out);
  buf buffer_1 (R_W_47630a0a, d_latch_33_not_q);
  nand L_23_d0835dd9 (L_1_PC_1c371e3f, d_latch_26_q, or_1_out);

  // Other names for the same wires on the sheet: L_ready_9a3f8f92 = L_READY_a37d69a3

  // Notes on the sheet:
  //   35
  //   16
  //   72
  //   /STORE
  //   14
  //   !!!
  //   7
  //   9
  //   70
  //   74
  //   78
  //   2
  //   10
  //   27
  //   26
  //   20
  //   ReadyDelay
  //   71
  //   TRES1
  //   22
  //   40
  //   8,1
  //   8,2
  //   56,1
  //   56,3
  //   56,2
  //   ACRL1
  //   !!!
  //   REST
  //   ENDS
  //   48
  //   ENDS
  //   RDY
  //   !!!
  //   ENDS
  //   50,1
  //   46
  //   4
  //   59
  //   42
  //   39
  //   WR
  //   26,2
  //   26,1
  //   29
  //   28
  //   53
  //   50,2
  //   49
  //   45
  //   7
  //   41
  //   67
  //   52
  //   23
  //   23,1
  //   23,2
  //   44
  //   55
  //   66
endmodule

// BUS CONTROL
module BUS_CONTROL (
  input  PHI1,
  input  PHI2,
  input  SBXY,
  input  D55,
  input  D57,
  input  D58,
  input  D59,
  input  D60,
  input  D61,
  input  D62,
  input  D63,
  input  D64,
  input  D65,
  input  D66,
  input  D67,
  input  D68,
  input  AND,
  input  D71,
  input  D72,
  input  D73,
  input  D74,
  input  D79,
  input  STOR,
  input  D81,
  input  D82,
  input  D84,
  input  D89,
  input  D90,
  input  D91,
  input  D83,
  input  D128,
  input  D129,
  input  L_0_ADL0_f8fabdab,
  input  BR2,
  input  ACRL2,
  input  DL_PCH_0dc37cb4,
  input  BR3,
  input  L_READY_a37d69a3,
  input  T2,
  input  INC_SB,
  input  D45,
  input  BRK6E,
  input  D46,
  input  D47,
  input  D48,
  input  STXY,
  input  D101,
  input  L_PCH_PCH_e0d9e687,
  input  T0,
  input  T1,
  input  T5,
  input  T6,
  input  D56,
  output L_0_ADH0_e340c71e,
  output L_0_ADH17_f181a8fa,
  output SB_AC_b159eec5,
  output ZTST,
  output ADL_ABL_5bea59e2,
  output AC_SB_c49f602a,
  output SB_DB_641efa5a,
  output AC_DB_519ce409,
  output PGX,
  output SB_ADH_4f1456ff,
  output DL_ADH_3839a3d0,
  output DL_ADL_6c5e0116,
  output ADH_ABH_8f72aca9,
  output DL_DB_69522204
);

  wire and_1_out, buffer_2_out, buffer_4_out, buffer_6_out, d_latch_1_not_q, d_latch_3_not_q,
       d_latch_4_not_q, d_latch_5_not_q, d_latch_6_not_q, d_latch_7_not_q, d_latch_8_not_q, d_latch_9_not_q,
       d_latch_10_not_q, d_latch_11_not_q, d_latch_12_not_q, d_latch_13_not_q, L_1_28cbbb7d_out,
       L_3_39a566ac_out, L_4_558283f2_out, L_5_9518e519_out, L_8_05eb4f56_out, L_9_0082242d_out,
       L_10_57b0d741_out, L_12_85a3418f_out, L_14_4f483598_out, L_15_5dad5732_out, L_25_f5ad6aee_out,
       L_27_6492a6f4_out, L_28_647e552a_out, L_31_e958c8e2_out, L_32_7de83e69_out, L_33_cae225fb_out,
       L_35_8b2262aa_out, L_36_34609549_out, L_37_acfb42d2_out, L_38_43aa51c3_out, L_40_1e6b68e0_out,
       L_41_b24af141_out, L_42_ae8bf3e0_out, L_43_fdaf143b_out, L_47_7c60183d_out, L_48_330a6f3f_out,
       L_49_f70f8148_out, nor_1_out, nor_2_out, nor_3_out, nor_4_out, nor_5_out, nor_6_out, nor_7_out,
       not_1_out, not_2_out, not_3_out, not_4_out, not_5_out, not_6_out, not_7_out, not_8_out, not_9_out,
       or_1_out;

  not not_1 (not_1_out, D64);
  nor L_40_1e6b68e0 (L_40_1e6b68e0_out, D71, D72);
  not not_2 (not_2_out, D73);
  and L_47_7c60183d (L_47_7c60183d_out, D79, STOR);
  nor L_48_330a6f3f (L_48_330a6f3f_out, D81, D82);
  nor nor_1 (nor_1_out, D90, D129);
  nor nor_2 (nor_2_out, D83, D129);
  nor nor_3 (nor_3_out, D128, D129);
  not not_3 (not_3_out, D48);
  nor L_36_34609549 (L_36_34609549_out, D58, D59, D60, D61, D62, D63, D64);
  and L_38_43aa51c3 (L_38_43aa51c3_out, not_1_out, D65);
  not not_4 (not_4_out, L_40_1e6b68e0_out);
  nand L_45_e516ed8c (PGX, L_40_1e6b68e0_out, not_2_out);
  nor nor_4 (nor_4_out, D74, L_47_7c60183d_out);
  nor L_49_f70f8148 (L_49_f70f8148_out, D89, nor_1_out, D91, D84);
  nor L_5_9518e519 (L_5_9518e519_out, nor_2_out, T0);
  D_Latch d_latch_1 (.NOT_Q(d_latch_1_not_q), .D(L_READY_a37d69a3), .EN(PHI1));  // open: Q
  nor L_1_28cbbb7d (L_1_28cbbb7d_out, INC_SB, D45, BRK6E, D46, D47, D48);
  not not_5 (not_5_out, L_36_34609549_out);
  nor L_37_acfb42d2 (L_37_acfb42d2_out, L_38_43aa51c3_out, AND);
  not not_6 (not_6_out, L_49_f70f8148_out);
  nor L_4_558283f2 (L_4_558283f2_out, L_5_9518e519_out, nor_3_out);
  nand L_14_4f483598 (L_14_4f483598_out, ACRL2, d_latch_1_not_q);
  not not_7 (not_7_out, L_1_28cbbb7d_out);
  nand L_27_6492a6f4 (L_27_6492a6f4_out, not_3_out, STXY);
  nor L_33_cae225fb (L_33_cae225fb_out, SBXY, not_5_out, T6, AND);
  nor L_43_fdaf143b (L_43_fdaf143b_out, not_4_out, L_READY_a37d69a3);
  nor L_12_85a3418f (L_12_85a3418f_out, PGX, BR3);
  nor L_10_57b0d741 (L_10_57b0d741_out, not_6_out, T2, L_PCH_PCH_e0d9e687, D56);
  nand L_28_647e552a (L_28_647e552a_out, T5, D55);
  not not_8 (not_8_out, L_28_647e552a_out);
  not not_9 (not_9_out, L_48_330a6f3f_out);
  nor L_15_5dad5732 (L_15_5dad5732_out, L_12_85a3418f_out, L_14_4f483598_out);
  nor L_9_0082242d (L_9_0082242d_out, L_READY_a37d69a3, L_10_57b0d741_out);
  nor L_35_8b2262aa (L_35_8b2262aa_out, D57, not_9_out);
  nor L_31_e958c8e2 (L_31_e958c8e2_out, L_33_cae225fb_out, AND);
  or or_1 (or_1_out, L_15_5dad5732_out, L_9_0082242d_out);
  nor L_41_b24af141 (L_41_b24af141_out, T6, T5);
  nand L_42_ae8bf3e0 (L_42_ae8bf3e0_out, L_41_b24af141_out, L_43_fdaf143b_out);
  nor L_32_7de83e69 (L_32_7de83e69_out, not_8_out, L_31_e958c8e2_out, D67, T1, BR2, L_27_6492a6f4_out);
  nor L_25_f5ad6aee (L_25_f5ad6aee_out, DL_PCH_0dc37cb4, not_6_out);
  nor L_8_05eb4f56 (L_8_05eb4f56_out, L_0_ADL0_f8fabdab, and_1_out);
  and and_1 (and_1_out, or_1_out, BR3);
  nor L_3_39a566ac (L_3_39a566ac_out, BR2, T5);
  D_Latch d_latch_2 (.NOT_Q(L_0_ADH0_e340c71e), .D(L_48_330a6f3f_out), .EN(PHI2));  // open: Q
  D_Latch d_latch_3 (.NOT_Q(d_latch_3_not_q), .D(L_35_8b2262aa_out), .EN(PHI2));  // open: Q
  D_Latch d_latch_4 (.NOT_Q(d_latch_4_not_q), .D(L_36_34609549_out), .EN(PHI2));  // open: Q
  D_Latch d_latch_5 (.NOT_Q(d_latch_5_not_q), .D(L_42_ae8bf3e0_out), .EN(PHI2));  // open: Q
  D_Latch d_latch_6 (.NOT_Q(d_latch_6_not_q), .D(L_37_acfb42d2_out), .EN(PHI2));  // open: Q
  D_Latch d_latch_7 (.NOT_Q(d_latch_7_not_q), .D(L_32_7de83e69_out), .EN(PHI2));  // open: Q
  D_Latch d_latch_8 (.NOT_Q(d_latch_8_not_q), .D(nor_4_out), .EN(PHI2));  // open: Q
  D_Latch d_latch_9 (.NOT_Q(d_latch_9_not_q), .D(L_12_85a3418f_out), .EN(PHI2));  // open: Q
  D_Latch d_latch_10 (.NOT_Q(d_latch_10_not_q), .D(L_25_f5ad6aee_out), .EN(PHI2));  // open: Q
  D_Latch d_latch_11 (.NOT_Q(d_latch_11_not_q), .D(L_48_330a6f3f_out), .EN(PHI2));  // open: Q
  D_Latch d_latch_12 (.NOT_Q(d_latch_12_not_q), .D(L_8_05eb4f56_out), .EN(PHI2));  // open: Q
  D_Latch d_latch_13 (.NOT_Q(d_latch_13_not_q), .D(L_3_39a566ac_out), .EN(PHI2));  // open: Q
  buf buffer_1 (L_0_ADH17_f181a8fa, d_latch_3_not_q);
  nor nor_5 (nor_5_out, PHI2, d_latch_4_not_q);
  buf buffer_2 (buffer_2_out, nor_5_out);
  not not_10 (ZTST, L_33_cae225fb_out);
  buf buffer_3 (ADL_ABL_5bea59e2, d_latch_5_not_q);
  nor nor_6 (nor_6_out, PHI2, d_latch_6_not_q);
  buf buffer_4 (buffer_4_out, nor_6_out);
  buf buffer_5 (SB_DB_641efa5a, d_latch_7_not_q);
  nor nor_7 (nor_7_out, PHI2, d_latch_8_not_q);
  buf buffer_6 (buffer_6_out, nor_7_out);
  buf buffer_7 (SB_ADH_4f1456ff, d_latch_9_not_q);
  buf buffer_8 (DL_ADH_3839a3d0, d_latch_10_not_q);
  buf buffer_9 (DL_ADL_6c5e0116, d_latch_11_not_q);
  buf buffer_10 (ADH_ABH_8f72aca9, d_latch_12_not_q);
  buf buffer_11 (DL_DB_69522204, d_latch_13_not_q);
  nor nor_8 (SB_AC_b159eec5, PHI2, buffer_2_out);
  nor nor_9 (AC_SB_c49f602a, PHI2, buffer_4_out);
  nor nor_10 (AC_DB_519ce409, PHI2, buffer_6_out);

  // Other names for the same wires on the sheet: L_ready_9a3f8f92 = L_READY_a37d69a3; RTS_5_475d8b78 = D84

  // Notes on the sheet:
  //   !!!
  //   BR0
  //   STA
  //   JSR2
  //   39
  //   46
  //   ABS/2
  //   IMPLED
  //   push/pull
  //   26
  //   44
  //   PGX
  //   #DL/ADL
  //   13
  //   #SB/AC
  //   33,1
  //   SBXY
  //   50
  //   IND
  //   2
  //   JSR/5
  //   #DL/ADL
  //   AND
  //   T2
  //   29
  //   34
  //   #ZTST
  //   SBA
  //   JSXY
  //   JMP/4
  //   JSXY
  //   #DL/ADL
  //   #SB/AC
  //   #ADL/ABL
  //   #AC/SB
  //   #SB/DB
  //   #DL/ADL
  //   #DL/DB
  //   19
  //   17
  //   7
  //   20
  //   16
  //   21
  //   18
  //   23
  //   22
  //   6
  //   24
endmodule

// FLAGS CONTROL
module FLAGS_CONTROL (
  input  PHI2,
  input  D98,
  input  D99,
  input  D108,
  input  D110,
  input  D120,
  input  D127,
  input  D107,
  input  T6,
  input  D112,
  input  D116,
  input  D117,
  input  D118,
  input  D119,
  input  ZTST,
  input  D109,
  input  L_READY_a37d69a3,
  input  SR,
  input  D114,
  input  D115,
  input  D113,
  output P_DB_42279b60,
  output IR5_I_e7eeeda5,
  output IR5_C_8cbf3e52,
  output IR5_D_ec89b364,
  output L_0_V_f0a8dd83,
  output ACR_C_5cb02b46,
  output DBZ_Z_a7859eb1,
  output DB_N_68ba26fc,
  output DB_P_37e5c1ba,
  output DB_C_01ed158e,
  output DB_V_92adf01b
);

  wire and_1_out, d_latch_7_q, d_latch_8_q, d_latch_10_q, d_latch_11_q, L_1_28cbbb7d_out, L_3_39a566ac_out,
       L_4_558283f2_out, L_9_0082242d_out, L_14_4f483598_out, L_15_5dad5732_out, L_21_ada5c31c_out,
       not_1_out, not_2_out, not_3_out, not_4_out;

  nor L_4_558283f2 (L_4_558283f2_out, D98, D99);
  not not_1 (not_1_out, D108);
  not not_2 (not_2_out, D110);
  not not_3 (not_3_out, D120);
  not L_9_0082242d (L_9_0082242d_out, D127);
  and and_1 (and_1_out, D107, T6);
  nor L_3_39a566ac (L_3_39a566ac_out, D114, D115);
  not not_4 (not_4_out, D113);
  nor L_1_28cbbb7d (L_1_28cbbb7d_out, and_1_out, D112, D116, D117, D118, D119);
  nor L_14_4f483598 (L_14_4f483598_out, ACR_C_5cb02b46, ZTST, D109);
  nor L_15_5dad5732 (L_15_5dad5732_out, SR, DB_P_37e5c1ba);
  D_Latch d_latch_1 (.NOT_Q(P_DB_42279b60), .D(L_4_558283f2_out), .EN(PHI2));  // open: Q
  D_Latch d_latch_2 (.NOT_Q(IR5_I_e7eeeda5), .D(not_1_out), .EN(PHI2));  // open: Q
  D_Latch d_latch_3 (.NOT_Q(IR5_C_8cbf3e52), .D(not_2_out), .EN(PHI2));  // open: Q
  D_Latch d_latch_4 (.NOT_Q(IR5_D_ec89b364), .D(not_3_out), .EN(PHI2));  // open: Q
  D_Latch d_latch_5 (.NOT_Q(L_0_V_f0a8dd83), .D(L_9_0082242d_out), .EN(PHI2));  // open: Q
  D_Latch d_latch_6 (.NOT_Q(ACR_C_5cb02b46), .D(L_1_28cbbb7d_out), .EN(PHI2));  // open: Q
  D_Latch d_latch_7 (.Q(d_latch_7_q), .NOT_Q(DBZ_Z_a7859eb1), .D(L_14_4f483598_out), .EN(PHI2));
  D_Latch d_latch_8 (.Q(d_latch_8_q), .D(D109), .EN(PHI2));  // open: NOT_Q
  D_Latch d_latch_9 (.NOT_Q(DB_C_01ed158e), .D(L_15_5dad5732_out), .EN(PHI2));  // open: Q
  D_Latch d_latch_10 (.Q(d_latch_10_q), .D(L_3_39a566ac_out), .EN(PHI2));  // open: NOT_Q
  D_Latch d_latch_11 (.Q(d_latch_11_q), .D(not_4_out), .EN(PHI2));  // open: NOT_Q
  and L_21_ada5c31c (L_21_ada5c31c_out, d_latch_7_q, d_latch_10_q);
  nor L_20_adeacd1b (DB_P_37e5c1ba, d_latch_10_q, L_READY_a37d69a3);
  nand L_12_85a3418f (DB_V_92adf01b, d_latch_10_q, d_latch_11_q);
  nor L_22_f545d19e (DB_N_68ba26fc, L_21_ada5c31c_out, d_latch_8_q);

  // Notes on the sheet:
  //   AVR/V
  //   BIT1
  //   BIT0
  //   /POUT
  //   2
  //   /CSI
  //   5
  //   19
  //   11
  //   /PIN
  //   /ARIT
  //   ZTST
  //   BIT1
  //   8
  //   7
  //   6
  //   18
  //   10
  //   13
  //   17
  //   22
  //   16
  //   12
  //   12,2
  //   21
  //   20
  //   21,1
endmodule

module FLAGS (
  input  P_DB_42279b60,
  input  B_OUT,
  input  DB0,
  input  in_4,
  input  in_5,
  input  DB3,
  input  in_7,
  input  in_8,
  input  DB6,
  input  DB7,
  input  DB_P_37e5c1ba,
  input  DBZ_Z_a7859eb1,
  input  DB_N_68ba26fc,
  input  IR5_C_8cbf3e52,
  input  ACR,
  input  DB_C_01ed158e,
  input  ACR_C_5cb02b46,
  input  IR5_D_ec89b364,
  input  PHI1,
  input  PHI2,
  input  L_IR5_9e15d54c,
  input  IR5_I_e7eeeda5,
  input  AVR,
  input  DB_V_92adf01b,
  input  D112,
  input  L_0_V_f0a8dd83,
  input  SO,
  output out_28,
  output DB1,
  output DB2,
  output out_31,
  output DB4,
  output DB5,
  output out_34,
  output out_35,
  output L_Z_OUT_2813b2ba,
  output L_N_OUT_10df9d15,
  output L_C_OUT_f91ece9c,
  output L_D_OUT_7d61c6e7,
  output L_I_OUT_6792f219,
  output L_V_OUT_959779aa
);

  wire and_1_out, and_2_out, and_3_out, and_4_out, and_5_out, d_latch_1_not_q, d_latch_2_not_q,
       d_latch_3_not_q, d_latch_4_q, d_latch_6_not_q, d_latch_8_not_q, d_latch_10_q, d_latch_12_q,
       d_latch_14_q, d_latch_16_q, d_latch_17_q, multiplexer_1_out, multiplexer_2_out, nand_1_out,
       nand_2_out, nand_3_out, nand_4_out, nand_5_out, nand_6_out, nand_7_out, nand_8_out, nand_9_out,
       nand_10_out, nand_11_out, nand_12_out, nand_13_out, nand_14_out, nand_15_out, nand_16_out, nor_1_out,
       nor_2_out, nor_3_out, nor_4_out, nor_5_out, nor_6_out, not_1_out, not_2_out, not_3_out, not_4_out,
       not_5_out, not_6_out, not_7_out, not_8_out, not_9_out, not_10_out, not_11_out, not_12_out, not_13_out,
       not_14_out, not_15_out, not_16_out, not_17_out, or_1_out;

  not not_1 (not_1_out, SO);
  D_Latch d_latch_1 (.NOT_Q(d_latch_1_not_q), .D(D112), .EN(PHI2));  // open: Q
  nor nor_1 (nor_1_out, DB0, in_4, in_5, DB3, in_7, in_8, DB6, DB7);
  not not_2 (not_2_out, in_4);
  not not_3 (not_3_out, nor_1_out);
  not not_4 (not_4_out, DB7);
  D_Latch d_latch_2 (.NOT_Q(d_latch_2_not_q), .D(not_1_out), .EN(PHI1));  // open: Q
  nand nand_1 (nand_1_out, not_2_out, DB_P_37e5c1ba);
  nand nand_2 (nand_2_out, not_3_out, DBZ_Z_a7859eb1);
  nand nand_3 (nand_3_out, not_4_out, DB_N_68ba26fc);
  not not_5 (not_5_out, ACR);
  not not_6 (not_6_out, DB0);
  nor nor_2 (nor_2_out, DB_C_01ed158e, IR5_C_8cbf3e52, ACR_C_5cb02b46);
  not not_7 (not_7_out, DB3);
  nor nor_3 (nor_3_out, IR5_D_ec89b364, DB_P_37e5c1ba);
  not not_8 (not_8_out, in_5);
  nor nor_4 (nor_4_out, DB_P_37e5c1ba, IR5_I_e7eeeda5);
  not not_9 (not_9_out, AVR);
  not not_10 (not_10_out, DB6);
  nor nor_5 (nor_5_out, DB_V_92adf01b, d_latch_1_not_q, d_latch_17_q);
  and and_1 (and_1_out, nand_1_out, nand_2_out);
  nand nand_4 (nand_4_out, L_IR5_9e15d54c, IR5_C_8cbf3e52);
  nand nand_5 (nand_5_out, not_5_out, ACR_C_5cb02b46);
  nand nand_6 (nand_6_out, not_6_out, DB_C_01ed158e);
  nand nand_7 (nand_7_out, nor_2_out, d_latch_10_q);
  nand nand_8 (nand_8_out, IR5_D_ec89b364, L_IR5_9e15d54c);
  nand nand_9 (nand_9_out, not_7_out, DB_P_37e5c1ba);
  nand nand_10 (nand_10_out, nor_3_out, d_latch_12_q);
  nand nand_11 (nand_11_out, L_IR5_9e15d54c, IR5_I_e7eeeda5);
  nand nand_12 (nand_12_out, not_8_out, DB_P_37e5c1ba);
  nand nand_13 (nand_13_out, nor_4_out, d_latch_14_q);
  nand nand_14 (nand_14_out, not_9_out, d_latch_1_not_q);
  nand nand_15 (nand_15_out, not_10_out, DB_V_92adf01b);
  nand nand_16 (nand_16_out, nor_5_out, d_latch_16_q);
  not not_11 (not_11_out, L_0_V_f0a8dd83);
  D_Latch d_latch_3 (.NOT_Q(d_latch_3_not_q), .D(d_latch_2_not_q), .EN(PHI2));  // open: Q
  or or_1 (or_1_out, DB_P_37e5c1ba, DBZ_Z_a7859eb1);
  and and_2 (and_2_out, nand_4_out, nand_5_out, nand_6_out, nand_7_out);
  and and_3 (and_3_out, nand_8_out, nand_9_out, nand_10_out);
  and and_4 (and_4_out, nand_11_out, nand_12_out, nand_13_out);
  and and_5 (and_5_out, nand_14_out, nand_15_out, nand_16_out, not_11_out);
  D_Latch d_latch_4 (.Q(d_latch_4_q), .D(d_latch_3_not_q), .EN(PHI1));  // open: NOT_Q
  Multiplexer multiplexer_1 (.in0(d_latch_6_not_q), .in1(and_1_out), .out(multiplexer_1_out), .sel(or_1_out));
  Multiplexer multiplexer_2 (.in0(d_latch_8_not_q), .in1(nand_3_out), .out(multiplexer_2_out), .sel(DB_N_68ba26fc));
  nor nor_6 (nor_6_out, d_latch_4_q, d_latch_2_not_q);
  D_Latch d_latch_5 (.NOT_Q(L_Z_OUT_2813b2ba), .D(multiplexer_1_out), .EN(PHI1));  // open: Q
  D_Latch d_latch_6 (.NOT_Q(d_latch_6_not_q), .D(L_Z_OUT_2813b2ba), .EN(PHI2));  // open: Q
  D_Latch d_latch_7 (.NOT_Q(L_N_OUT_10df9d15), .D(multiplexer_2_out), .EN(PHI1));  // open: Q
  D_Latch d_latch_8 (.NOT_Q(d_latch_8_not_q), .D(L_N_OUT_10df9d15), .EN(PHI2));  // open: Q
  D_Latch d_latch_9 (.NOT_Q(L_C_OUT_f91ece9c), .D(and_2_out), .EN(PHI1));  // open: Q
  D_Latch d_latch_10 (.Q(d_latch_10_q), .D(L_C_OUT_f91ece9c), .EN(PHI2));  // open: NOT_Q
  D_Latch d_latch_11 (.NOT_Q(L_D_OUT_7d61c6e7), .D(and_3_out), .EN(PHI1));  // open: Q
  D_Latch d_latch_12 (.Q(d_latch_12_q), .D(L_D_OUT_7d61c6e7), .EN(PHI2));  // open: NOT_Q
  D_Latch d_latch_13 (.NOT_Q(L_I_OUT_6792f219), .D(and_4_out), .EN(PHI1));  // open: Q
  D_Latch d_latch_14 (.Q(d_latch_14_q), .D(L_I_OUT_6792f219), .EN(PHI2));  // open: NOT_Q
  D_Latch d_latch_15 (.NOT_Q(L_V_OUT_959779aa), .D(and_5_out), .EN(PHI1));  // open: Q
  D_Latch d_latch_16 (.Q(d_latch_16_q), .D(L_V_OUT_959779aa), .EN(PHI2));  // open: NOT_Q
  D_Latch d_latch_17 (.Q(d_latch_17_q), .D(nor_6_out), .EN(PHI2));  // open: NOT_Q
  not not_12 (not_12_out, L_C_OUT_f91ece9c);
  assign out_28 = P_DB_42279b60 ? not_12_out : 1'bz;  // Controlled_Buffer controlled_buffer_1
  not not_13 (not_13_out, L_Z_OUT_2813b2ba);
  assign DB1 = P_DB_42279b60 ? not_13_out : 1'bz;  // Controlled_Buffer controlled_buffer_2
  not not_14 (not_14_out, L_I_OUT_6792f219);
  assign DB2 = P_DB_42279b60 ? not_14_out : 1'bz;  // Controlled_Buffer controlled_buffer_3
  not not_15 (not_15_out, L_D_OUT_7d61c6e7);
  assign out_31 = P_DB_42279b60 ? not_15_out : 1'bz;  // Controlled_Buffer controlled_buffer_4
  assign DB4 = P_DB_42279b60 ? B_OUT : 1'bz;  // Controlled_Buffer controlled_buffer_5
  not not_16 (not_16_out, L_V_OUT_959779aa);
  assign out_34 = P_DB_42279b60 ? not_16_out : 1'bz;  // Controlled_Buffer controlled_buffer_6
  not not_17 (not_17_out, L_N_OUT_10df9d15);
  assign out_35 = P_DB_42279b60 ? not_17_out : 1'bz;  // Controlled_Buffer controlled_buffer_7

  // Other names for the same wires on the sheet: DB2_t = in_5

  // Notes on the sheet:
  //   ACR/C
  //   AVR/V
  //   /DB1
  //   /DBZ
  //   /DB7
  //   DB/C
  //   IR5/D
  //   IR5/I
  //   DB/V
  //   1/V
  //   IR5/C
  //   /ACR
  //   ACR/C
  //   /DB0
  //   DB/C
  //   IR5/D
  //   /DB3
  //   IR5/I
  //   /DB2
  //   /AVR
  //   AVR/V
  //   /DB6
  //   DB/V
  //   0/V
  //   V FLAG
  //   Z FLAG
  //   /Z_OUT
  //   N FLAG
  //   /N_OUT
  //   C FLAG
  //   /C_OUT
  //   D FLAG
  //   /D_OUT
  //   I FLAG
  //   /I_OUT
  //   /V_OUT
  //   N.C.
endmodule

module ABL (
  input  PHI1,
  input  PHI2,
  input  ADL_ABL,
  input  L_0_ADL0,
  input  L_0_ADL1,
  input  L_0_ADL2,
  input  ADL0,
  input  ADL1,
  input  ADL2,
  input  ADL3,
  input  ADL4,
  input  ADL5,
  input  ADL6,
  input  ADL7,
  output A0,
  output A1,
  output A2,
  output A3,
  output A4,
  output A5,
  output A6,
  output A7
);

  ABL_LOW_BIT _0 (
    .Ax(A0), .ADL_ABL_5bea59e2(ADL_ABL), .L_0_ADLx_7ec67910(L_0_ADL0), .ADLx(ADL0), .PHI1(PHI1), .PHI2(PHI2));
  ABL_LOW_BIT _1 (
    .Ax(A1), .ADL_ABL_5bea59e2(ADL_ABL), .L_0_ADLx_7ec67910(L_0_ADL1), .ADLx(ADL1), .PHI1(PHI1), .PHI2(PHI2));
  ABL_LOW_BIT _2 (
    .Ax(A2), .ADL_ABL_5bea59e2(ADL_ABL), .L_0_ADLx_7ec67910(L_0_ADL2), .ADLx(ADL2), .PHI1(PHI1), .PHI2(PHI2));
  ABL_BIT _3 (.Ax(A3), .ADL_ABL_5bea59e2(ADL_ABL), .ADLx(ADL3), .PHI1(PHI1), .PHI2(PHI2));
  ABL_BIT _4 (.Ax(A4), .ADL_ABL_5bea59e2(ADL_ABL), .ADLx(ADL4), .PHI1(PHI1), .PHI2(PHI2));
  ABL_BIT _5 (.Ax(A5), .ADL_ABL_5bea59e2(ADL_ABL), .ADLx(ADL5), .PHI1(PHI1), .PHI2(PHI2));
  ABL_BIT _6 (.Ax(A6), .ADL_ABL_5bea59e2(ADL_ABL), .ADLx(ADL6), .PHI1(PHI1), .PHI2(PHI2));
  ABL_BIT _7 (.Ax(A7), .ADL_ABL_5bea59e2(ADL_ABL), .ADLx(ADL7), .PHI1(PHI1), .PHI2(PHI2));
endmodule

module REGS_BIT (
  input  PHI2,
  input  Y_SB,
  input  SB_Y,
  input  X_SB,
  input  SB_X,
  input  S_ADL,
  input  S_S,
  input  SB_S,
  input  S_SB,
  input  SBx_In,
  output SBx_Out,
  output ADLx,
  output Y_Debug,
  output X_Debug,
  output S_Debug
);

  wire and_1_out, and_2_out, and_3_out, not_1_out, not_2_out, not_3_out;

  not not_1 (not_1_out, PHI2);
  not not_2 (not_2_out, PHI2);
  not not_3 (not_3_out, PHI2);
  and and_1 (and_1_out, not_1_out, SB_Y);
  and and_2 (and_2_out, not_2_out, SB_X);
  and and_3 (and_3_out, not_3_out, SB_S);
  D_Flip_Flop #(.trigger("high")) Y (.D(SBx_In), .clk(and_1_out), .Q(Y_Debug));  // open: Qn, preset, reset
  D_Flip_Flop #(.trigger("high")) X (.D(SBx_In), .clk(and_2_out), .Q(X_Debug));  // open: Qn, preset, reset
  D_Flip_Flop #(.trigger("high")) S (.D(SBx_In), .clk(and_3_out), .Q(S_Debug));  // open: Qn, preset, reset
  assign SBx_Out = Y_SB ? Y_Debug : 1'bz;  // Controlled_Buffer controlled_buffer_1
  assign SBx_Out = X_SB ? X_Debug : 1'bz;  // Controlled_Buffer controlled_buffer_2
  assign SBx_Out = S_SB ? S_Debug : 1'bz;  // Controlled_Buffer controlled_buffer_3
  assign ADLx = S_ADL ? S_Debug : 1'bz;  // Controlled_Buffer controlled_buffer_4

  // Notes on the sheet:
  //   unused
endmodule

module REGS (
  input  PHI2,
  input  Y_SB,
  input  SB_Y,
  input  X_SB,
  input  SB_X,
  input  S_ADL,
  input  S_S,
  input  SB_S,
  input  S_SB,
  input  SB0_In,
  input  SB1_In,
  input  SB2_In,
  input  SB3_In,
  input  SB4_In,
  input  SB5_In,
  input  SB6_In,
  input  SB7_In,
  output SB0_Out,
  output SB1_Out,
  output SB2_Out,
  output SB3_Out,
  output SB4_Out,
  output SB5_Out,
  output SB6_Out,
  output SB7_Out,
  output ADL0,
  output ADL1,
  output ADL2,
  output ADL3,
  output ADL4,
  output ADL5,
  output ADL6,
  output ADL7,
  output [7:0] S_Debug,
  output [7:0] Y_Debug,
  output [7:0] X_Debug
);

  REGS_BIT _0 (
    .ADLx(ADL0), .Y_Debug(Y_Debug[0]), .X_Debug(X_Debug[0]), .S_Debug(S_Debug[0]), .SBx_Out(SB0_Out),
    .Y_SB(Y_SB), .SB_Y(SB_Y), .X_SB(X_SB), .SB_X(SB_X), .S_ADL(S_ADL), .S_S(S_S), .SB_S(SB_S), .S_SB(S_SB),
    .SBx_In(SB0_In), .PHI2(PHI2));
  REGS_BIT _4 (
    .ADLx(ADL4), .Y_Debug(Y_Debug[4]), .X_Debug(X_Debug[4]), .S_Debug(S_Debug[4]), .SBx_Out(SB4_Out),
    .Y_SB(Y_SB), .SB_Y(SB_Y), .X_SB(X_SB), .SB_X(SB_X), .S_ADL(S_ADL), .S_S(S_S), .SB_S(SB_S), .S_SB(S_SB),
    .SBx_In(SB4_In), .PHI2(PHI2));
  REGS_BIT _1 (
    .ADLx(ADL1), .Y_Debug(Y_Debug[1]), .X_Debug(X_Debug[1]), .S_Debug(S_Debug[1]), .SBx_Out(SB1_Out),
    .Y_SB(Y_SB), .SB_Y(SB_Y), .X_SB(X_SB), .SB_X(SB_X), .S_ADL(S_ADL), .S_S(S_S), .SB_S(SB_S), .S_SB(S_SB),
    .SBx_In(SB1_In), .PHI2(PHI2));
  REGS_BIT _5 (
    .ADLx(ADL5), .Y_Debug(Y_Debug[5]), .X_Debug(X_Debug[5]), .S_Debug(S_Debug[5]), .SBx_Out(SB5_Out),
    .Y_SB(Y_SB), .SB_Y(SB_Y), .X_SB(X_SB), .SB_X(SB_X), .S_ADL(S_ADL), .S_S(S_S), .SB_S(SB_S), .S_SB(S_SB),
    .SBx_In(SB5_In), .PHI2(PHI2));
  REGS_BIT _2 (
    .ADLx(ADL2), .Y_Debug(Y_Debug[2]), .X_Debug(X_Debug[2]), .S_Debug(S_Debug[2]), .SBx_Out(SB2_Out),
    .Y_SB(Y_SB), .SB_Y(SB_Y), .X_SB(X_SB), .SB_X(SB_X), .S_ADL(S_ADL), .S_S(S_S), .SB_S(SB_S), .S_SB(S_SB),
    .SBx_In(SB2_In), .PHI2(PHI2));
  REGS_BIT _6 (
    .ADLx(ADL6), .Y_Debug(Y_Debug[6]), .X_Debug(X_Debug[6]), .S_Debug(S_Debug[6]), .SBx_Out(SB6_Out),
    .Y_SB(Y_SB), .SB_Y(SB_Y), .X_SB(X_SB), .SB_X(SB_X), .S_ADL(S_ADL), .S_S(S_S), .SB_S(SB_S), .S_SB(S_SB),
    .SBx_In(SB6_In), .PHI2(PHI2));
  REGS_BIT _3 (
    .ADLx(ADL3), .Y_Debug(Y_Debug[3]), .X_Debug(X_Debug[3]), .S_Debug(S_Debug[3]), .SBx_Out(SB3_Out),
    .Y_SB(Y_SB), .SB_Y(SB_Y), .X_SB(X_SB), .SB_X(SB_X), .S_ADL(S_ADL), .S_S(S_S), .SB_S(SB_S), .S_SB(S_SB),
    .SBx_In(SB3_In), .PHI2(PHI2));
  REGS_BIT _7 (
    .ADLx(ADL7), .Y_Debug(Y_Debug[7]), .X_Debug(X_Debug[7]), .S_Debug(S_Debug[7]), .SBx_Out(SB7_Out),
    .Y_SB(Y_SB), .SB_Y(SB_Y), .X_SB(X_SB), .SB_X(SB_X), .S_ADL(S_ADL), .S_S(S_S), .SB_S(SB_S), .S_SB(S_SB),
    .SBx_In(SB7_In), .PHI2(PHI2));

  // Other names for the same wires on the sheet: S_ADL_07acd992 = S_ADL; S_S_09f08a69 = S_S; S_SB_e37affed = S_SB;
  //   SB_S_4c94ee46 = SB_S; SB_X_cf392641 = SB_X; SB_Y_9a33ae5e = SB_Y; X_SB_222038db = X_SB; Y_SB_d628d28f = Y_SB
endmodule

module DL_BIT (
  input  PHI1,
  input  PHI2,
  input  DL_ADL,
  input  DL_ADH,
  input  DL_DB,
  input  RD,
  input  in_7,
  input  Dx,
  output ADLx,
  output ADHx,
  output DBx,
  output out_12,
  output DOR_Debug,
  output DL_Debug
);

  wire and_1_out, and_2_out, and_3_out, not_1_out, not_2_out, not_3_out;

  D_Latch DL (.NOT_Q(DL_Debug), .D(not_1_out), .EN(PHI2));  // open: Q
  not not_1 (not_1_out, Dx);
  D_Latch DOR (.NOT_Q(DOR_Debug), .D(not_2_out), .EN(PHI1));  // open: Q
  not not_2 (not_2_out, in_7);
  and and_1 (and_1_out, DL_ADL, PHI1);
  and and_2 (and_2_out, DL_ADH, PHI1);
  and and_3 (and_3_out, DL_DB, PHI1);
  not not_3 (not_3_out, RD);
  assign ADLx = and_1_out ? DL_Debug : 1'bz;  // Controlled_Buffer controlled_buffer_1
  assign ADHx = and_2_out ? DL_Debug : 1'bz;  // Controlled_Buffer controlled_buffer_2
  assign DBx = and_3_out ? DL_Debug : 1'bz;  // Controlled_Buffer controlled_buffer_3
  assign out_12 = not_3_out ? DOR_Debug : 1'bz;  // Controlled_Buffer controlled_buffer_4
endmodule

module DL (
  input  PHI1,
  input  PHI2,
  input  WR,
  input  DL_ADL_6c5e0116,
  input  DL_ADH_3839a3d0,
  input  DL_DB_69522204,
  input  in_7,
  input  in_8,
  input  DB2,
  input  in_10,
  input  in_11,
  input  DB5,
  input  DB6,
  input  DB7,
  input  in_15,
  input  D1,
  input  in_17,
  input  D3,
  input  D4,
  input  in_20,
  input  in_21,
  input  in_22,
  output DB0,
  output DB1,
  output out_25,
  output DB3,
  output DB4,
  output out_28,
  output out_29,
  output out_30,
  output ADL0,
  output ADL1,
  output ADL2,
  output ADL3,
  output ADL4,
  output ADL5,
  output ADL6,
  output ADL7,
  output ADH0,
  output ADH1,
  output ADH2,
  output ADH3,
  output ADH4,
  output ADH5,
  output ADH6,
  output ADH7,
  output D0,
  output out_48,
  output D2,
  output out_50,
  output out_51,
  output D5,
  output D6,
  output D7,
  output [7:0] DL_Debug,
  output [7:0] DOR_Debug
);

  wire d_latch_1_not_q, RD;

  D_Latch d_latch_1 (.NOT_Q(d_latch_1_not_q), .D(WR), .EN(PHI1));  // open: Q
  Multiplexer multiplexer_1 (.in0(d_latch_1_not_q), .in1(1'b1), .out(RD), .sel(PHI2));
  DL_BIT _0 (
    .ADLx(ADL0), .ADHx(ADH0), .DBx(DB0), .out_12(D0), .DOR_Debug(DOR_Debug[0]), .DL_Debug(DL_Debug[0]),
    .DL_ADL(DL_ADL_6c5e0116), .DL_ADH(DL_ADH_3839a3d0), .DL_DB(DL_DB_69522204), .RD(RD), .in_7(in_7),
    .Dx(in_15), .PHI1(PHI1), .PHI2(PHI2));
  DL_BIT _1 (
    .ADLx(ADL1), .ADHx(ADH1), .DBx(DB1), .out_12(out_48), .DOR_Debug(DOR_Debug[1]), .DL_Debug(DL_Debug[1]),
    .DL_ADL(DL_ADL_6c5e0116), .DL_ADH(DL_ADH_3839a3d0), .DL_DB(DL_DB_69522204), .RD(RD), .in_7(in_8),
    .Dx(D1), .PHI1(PHI1), .PHI2(PHI2));
  DL_BIT _2 (
    .ADLx(ADL2), .ADHx(ADH2), .DBx(out_25), .out_12(D2), .DOR_Debug(DOR_Debug[2]), .DL_Debug(DL_Debug[2]),
    .DL_ADL(DL_ADL_6c5e0116), .DL_ADH(DL_ADH_3839a3d0), .DL_DB(DL_DB_69522204), .RD(RD), .in_7(DB2),
    .Dx(in_17), .PHI1(PHI1), .PHI2(PHI2));
  DL_BIT _3 (
    .ADLx(ADL3), .ADHx(ADH3), .DBx(DB3), .out_12(out_50), .DOR_Debug(DOR_Debug[3]), .DL_Debug(DL_Debug[3]),
    .DL_ADL(DL_ADL_6c5e0116), .DL_ADH(DL_ADH_3839a3d0), .DL_DB(DL_DB_69522204), .RD(RD), .in_7(in_10),
    .Dx(D3), .PHI1(PHI1), .PHI2(PHI2));
  DL_BIT _4 (
    .ADLx(ADL4), .ADHx(ADH4), .DBx(DB4), .out_12(out_51), .DOR_Debug(DOR_Debug[4]), .DL_Debug(DL_Debug[4]),
    .DL_ADL(DL_ADL_6c5e0116), .DL_ADH(DL_ADH_3839a3d0), .DL_DB(DL_DB_69522204), .RD(RD), .in_7(in_11),
    .Dx(D4), .PHI1(PHI1), .PHI2(PHI2));
  DL_BIT _5 (
    .ADLx(ADL5), .ADHx(ADH5), .DBx(out_28), .out_12(D5), .DOR_Debug(DOR_Debug[5]), .DL_Debug(DL_Debug[5]),
    .DL_ADL(DL_ADL_6c5e0116), .DL_ADH(DL_ADH_3839a3d0), .DL_DB(DL_DB_69522204), .RD(RD), .in_7(DB5),
    .Dx(in_20), .PHI1(PHI1), .PHI2(PHI2));
  DL_BIT _6 (
    .ADLx(ADL6), .ADHx(ADH6), .DBx(out_29), .out_12(D6), .DOR_Debug(DOR_Debug[6]), .DL_Debug(DL_Debug[6]),
    .DL_ADL(DL_ADL_6c5e0116), .DL_ADH(DL_ADH_3839a3d0), .DL_DB(DL_DB_69522204), .RD(RD), .in_7(DB6),
    .Dx(in_21), .PHI1(PHI1), .PHI2(PHI2));
  DL_BIT _7 (
    .ADLx(ADL7), .ADHx(ADH7), .DBx(out_30), .out_12(D7), .DOR_Debug(DOR_Debug[7]), .DL_Debug(DL_Debug[7]),
    .DL_ADL(DL_ADL_6c5e0116), .DL_ADH(DL_ADH_3839a3d0), .DL_DB(DL_DB_69522204), .RD(RD), .in_7(DB7),
    .Dx(in_22), .PHI1(PHI1), .PHI2(PHI2));
endmodule

module ALU (
  input  PHI2,
  input  NDB_ADD_ee0a1870,
  input  DB_ADD_48d85b7e,
  input  L_0_ADD_81d17e61,
  input  SB_ADD_0eab26ac,
  input  ADL_ADD_e28b8a30,
  input  ADD_SB06_a3738230,
  input  ADD_SB7_a8f4b77a,
  input  ADD_ADL_3fac4345,
  input  ANDS,
  input  EORS,
  input  ORS,
  input  SRS,
  input  SUMS,
  input  SB_AC_b159eec5,
  input  AC_SB_c49f602a,
  input  AC_DB_519ce409,
  input  SB_DB_641efa5a,
  input  SB_ADH_4f1456ff,
  input  L_0_ADH0_e340c71e,
  input  L_0_ADH17_f181a8fa,
  input  L_ACIN_e173f520,
  input  L_DAA_82b80d94,
  input  L_DSA_ea96e89b,
  input  SB0,
  input  in_26,
  input  ADL0,
  input  in_28,
  input  DB1,
  input  ADL1,
  input  SB2,
  input  in_32,
  input  in_33,
  input  SB3,
  input  in_35,
  input  ADL3,
  input  in_37,
  input  in_38,
  input  in_39,
  input  SB5,
  input  DB5,
  input  ADL5,
  input  SB6,
  input  DB6,
  input  in_45,
  input  in_46,
  input  in_47,
  input  ADL7,
  output ACR,
  output AVR,
  output [7:0] ADD_Debug,
  output [7:0] AC_Debug,
  output [7:0] AI_Debug,
  output [7:0] BI_Debug,
  output out_55,
  output DB0,
  output out_57,
  output ADH0,
  output SB1,
  output out_60,
  output out_61,
  output ADH1,
  output out_63,
  output DB2,
  output ADL2,
  output ADH2,
  output out_67,
  output DB3,
  output out_69,
  output ADH3,
  output SB4,
  output DB4,
  output ADL4,
  output ADH4,
  output out_75,
  output out_76,
  output out_77,
  output ADH5,
  output out_79,
  output out_80,
  output ADL6,
  output ADH6,
  output SB7,
  output DB7,
  output out_85,
  output ADH7
);

  wire ACLatch_q, alu_ops_1_carry4, alu_ops_1_carry6, alu_ops_1_l_carry3_9e435978,
       alu_ops_1_l_carry7_b3181e70, and_1_out, bcd_carry_1_dc3, bcd_carry_1_dc7, DCLatch_q, nand_1_out,
       nor_1_out, nor_2_out, not_1_out, not_2_out;
  wire [7:0] alu_add_1_l_addx_85db8c05, alu_bcd_1_out0, alu_ops_1_nand0, alu_ops_1_nor0, alu_ops_1_res0,
       alu_ops_1_xor0;

  ALU_OPS alu_ops_1 (
    .BI_Debug(BI_Debug), .L_carry3_9e435978(alu_ops_1_l_carry3_9e435978),
    .L_carry7_b3181e70(alu_ops_1_l_carry7_b3181e70), .xor2(alu_ops_1_xor0[2]), .xor3(alu_ops_1_xor0[3]),
    .xor4(alu_ops_1_xor0[4]), .xor5(alu_ops_1_xor0[5]), .xor6(alu_ops_1_xor0[6]), .xor7(alu_ops_1_xor0[7]),
    .res0(alu_ops_1_res0[0]), .res1(alu_ops_1_res0[1]), .res2(alu_ops_1_res0[2]), .res3(alu_ops_1_res0[3]),
    .res4(alu_ops_1_res0[4]), .res5(alu_ops_1_res0[5]), .res6(alu_ops_1_res0[6]), .res7(alu_ops_1_res0[7]),
    .carry4(alu_ops_1_carry4), .nor0(alu_ops_1_nor0[0]), .nor1(alu_ops_1_nor0[1]), .nor2(alu_ops_1_nor0[2]),
    .nor3(alu_ops_1_nor0[3]), .nor4(alu_ops_1_nor0[4]), .nor5(alu_ops_1_nor0[5]), .nor6(alu_ops_1_nor0[6]),
    .nor7(alu_ops_1_nor0[7]), .nand0(alu_ops_1_nand0[0]), .carry6(alu_ops_1_carry6),
    .nand1(alu_ops_1_nand0[1]), .nand2(alu_ops_1_nand0[2]), .nand3(alu_ops_1_nand0[3]),
    .nand4(alu_ops_1_nand0[4]), .nand5(alu_ops_1_nand0[5]), .nand6(alu_ops_1_nand0[6]),
    .nand7(alu_ops_1_nand0[7]), .xor0(alu_ops_1_xor0[0]), .xor1(alu_ops_1_xor0[1]), .AI_Debug(AI_Debug),
    .DB_ADD_48d85b7e(DB_ADD_48d85b7e), .DB5(DB5), .DB6(DB6), .DB7(in_47), .ADL0(ADL0), .ADL1(ADL1),
    .ADL2(in_33), .ADL3(ADL3), .ADL4(in_39), .ADL5(ADL5), .L_0_ADD_81d17e61(L_0_ADD_81d17e61), .ADL6(in_45),
    .ADL7(ADL7), .SB_ADD_0eab26ac(SB_ADD_0eab26ac), .ADL_ADD_e28b8a30(ADL_ADD_e28b8a30), .ANDS(ANDS),
    .EORS(EORS), .ORS(ORS), .SRS(SRS), .SUMS(SUMS), .L_cin_af3836dd(L_ACIN_e173f520), .DC3(bcd_carry_1_dc3),
    .SB0(SB0), .SB1(in_28), .SB2(SB2), .SB3(SB3), .NDB_ADD_ee0a1870(NDB_ADD_ee0a1870), .SB4(in_37),
    .SB5(SB5), .SB6(SB6), .SB7(in_46), .DB0(in_26), .DB1(DB1), .DB2(in_32), .DB3(in_35), .DB4(in_38));
  BCD_CARRY bcd_carry_1 (
    .DC3(bcd_carry_1_dc3), .DC7(bcd_carry_1_dc7), .L_ACIN_e173f520(L_ACIN_e173f520),
    .carry4(alu_ops_1_carry4), .L_DAA_82b80d94(L_DAA_82b80d94), .\nor (alu_ops_1_nor0),
    .\nand (alu_ops_1_nand0), .\xor (alu_ops_1_xor0));
  nand nand_1 (nand_1_out, alu_ops_1_carry6, alu_ops_1_nor0[7]);
  nor nor_1 (nor_1_out, alu_ops_1_carry6, alu_ops_1_l_carry7_b3181e70);
  not not_1 (not_1_out, nor_1_out);
  ALU_ADD alu_add_1 (
    .L_ADDx_85db8c05(alu_add_1_l_addx_85db8c05), .SB0(out_55), .SB1(SB1), .SB2(out_63), .SB3(out_67),
    .SB4(SB4), .SB5(out_75), .SB6(out_79), .SB7(SB7), .ADL0(out_57), .ADL1(out_61), .ADL2(ADL2),
    .ADL3(out_69), .ADL4(ADL4), .ADL5(out_77), .ADL6(ADL6), .ADL7(out_85), .ADD_Debug(ADD_Debug),
    .ADD_SB06_a3738230(ADD_SB06_a3738230), .ADD_SB7_a8f4b77a(ADD_SB7_a8f4b77a),
    .ADD_ADL_3fac4345(ADD_ADL_3fac4345), .PHI2(PHI2), .L_res_da3ec8b2(alu_ops_1_res0));
  D_Latch DCLatch (.Q(DCLatch_q), .D(bcd_carry_1_dc7), .EN(PHI2));  // open: NOT_Q
  D_Latch ACLatch (.Q(ACLatch_q), .D(not_2_out), .EN(PHI2));  // open: NOT_Q
  not not_2 (not_2_out, alu_ops_1_l_carry7_b3181e70);
  D_Latch AVRLatch (.NOT_Q(AVR), .D(and_1_out), .EN(PHI2));  // open: Q
  and and_1 (and_1_out, nand_1_out, not_1_out);
  nor nor_2 (nor_2_out, DCLatch_q, ACLatch_q);
  not not_3 (ACR, nor_2_out);
  ALU_BCD alu_bcd_1 (
    .out0(alu_bcd_1_out0[0]), .out1(alu_bcd_1_out0[1]), .out2(alu_bcd_1_out0[2]), .out3(alu_bcd_1_out0[3]),
    .out4(alu_bcd_1_out0[4]), .out5(alu_bcd_1_out0[5]), .out6(alu_bcd_1_out0[6]), .out7(alu_bcd_1_out0[7]),
    .L_carry3_9e435978(alu_ops_1_l_carry3_9e435978), .ACR(ACR), .L_DAA_82b80d94(L_DAA_82b80d94),
    .L_DSA_ea96e89b(L_DSA_ea96e89b), .SB0(SB0), .SB1(in_28), .SB2(SB2), .SB3(SB3), .SB4(in_37), .SB5(SB5),
    .SB6(SB6), .PHI2(PHI2), .SB7(in_46), .L_ADDx_85db8c05(alu_add_1_l_addx_85db8c05));
  ALU_AC alu_ac_1 (
    .AC_Debug(AC_Debug), .SB1(SB1), .out_21(out_63), .SB3(out_67), .out_23(SB4), .out_24(out_75),
    .out_25(out_79), .SB7(SB7), .ADH0(ADH0), .ADH1(ADH1), .ADH2(ADH2), .ADH3(ADH3), .ADH4(ADH4), .ADH5(ADH5),
    .out_19(out_55), .ADH6(ADH6), .ADH7(ADH7), .DB0(DB0), .DB1(out_60), .DB2(DB2), .DB3(DB3), .DB4(DB4),
    .DB5(out_76), .DB6(out_80), .DB7(DB7), .SB_AC_b159eec5(SB_AC_b159eec5), .AC_SB_c49f602a(AC_SB_c49f602a),
    .AC_DB_519ce409(AC_DB_519ce409), .SB_DB_641efa5a(SB_DB_641efa5a), .SB_ADH_4f1456ff(SB_ADH_4f1456ff),
    .L_0_ADH0_e340c71e(L_0_ADH0_e340c71e), .L_0_ADH17_f181a8fa(L_0_ADH17_f181a8fa), .SB0(SB0), .in_11(in_28),
    .SB2(SB2), .in_13(SB3), .SB4(in_37), .SB5(SB5), .SB6(SB6), .in_17(in_46), .PHI2(PHI2),
    .ins(alu_bcd_1_out0));

  // Notes on the sheet:
  //   x8
  //   AVR
  //   ACR
  //   x8
  //   x8
endmodule

module PC (
  input  PHI2,
  input  ADL_PCL_9a95c372,
  input  PCL_PCL_4f350f4d,
  input  PCL_ADL_ee043dbc,
  input  PCL_DB_4172714e,
  input  ADH_PCH_61520abf,
  input  PCH_PCH_807b9fbd,
  input  PCH_ADH_ead93594,
  input  PCH_DB_a81fefa0,
  input  L_1_PC_f2b91046,
  input  in_11,
  input  ADL1,
  input  ADL2,
  input  ADL3,
  input  ADL4,
  input  ADL5,
  input  in_17,
  input  ADL7,
  input  in_19,
  input  in_20,
  input  in_21,
  input  ADH3,
  input  in_23,
  input  in_24,
  input  in_25,
  input  in_26,
  output DB0,
  output DB1,
  output DB2,
  output DB3,
  output DB4,
  output DB5,
  output DB6,
  output DB7,
  output ADL0,
  output out_36,
  output out_37,
  output out_38,
  output out_39,
  output out_40,
  output ADL6,
  output out_42,
  output ADH0,
  output ADH1,
  output ADH2,
  output out_46,
  output ADH4,
  output ADH5,
  output ADH6,
  output ADH7,
  output [15:0] PC_Debug,
  output [15:0] PCS_Debug
);

  wire pcl_1_pclc;

  PCL pcl_1 (
    .PCL_Debug(PC_Debug[7:0]), .PCLS_Debug(PCS_Debug[7:0]), .ADL0(ADL0), .ADL1(out_36), .out_17(out_37),
    .ADL3(out_38), .out_19(out_39), .ADL5(out_40), .out_21(ADL6), .ADL7(out_42), .DB0(DB0), .DB1(DB1),
    .DB2(DB2), .DB3(DB3), .DB4(DB4), .DB5(DB5), .DB6(DB6), .DB7(DB7), .PCLC(pcl_1_pclc),
    .cin(L_1_PC_f2b91046), .ADL_PCL_9a95c372(ADL_PCL_9a95c372), .PCL_PCL_4f350f4d(PCL_PCL_4f350f4d),
    .PCL_ADL_ee043dbc(PCL_ADL_ee043dbc), .PCL_DB_4172714e(PCL_DB_4172714e), .PHI2(PHI2), .in_7(in_11),
    .in_8(ADL1), .ADL2(ADL2), .in_10(ADL3), .ADL4(ADL4), .in_12(ADL5), .ADL6(in_17), .in_14(ADL7));
  PCH pch_1 (
    .ADH0(ADH0), .out_16(ADH1), .out_17(ADH2), .out_18(out_46), .out_19(ADH4), .out_20(ADH5), .ADH6(ADH6),
    .ADH7(ADH7), .DB0(DB0), .DB1(DB1), .DB2(DB2), .DB3(DB3), .DB4(DB4), .DB5(DB5), .DB6(DB6), .DB7(DB7),
    .PCH_Debug(PC_Debug[15:8]), .PCHS_Debug(PCS_Debug[15:8]), .cin(pcl_1_pclc),
    .ADH_PCH_61520abf(ADH_PCH_61520abf), .PCH_PCH_807b9fbd(PCH_PCH_807b9fbd),
    .PCH_ADH_ead93594(PCH_ADH_ead93594), .PCH_DB_a81fefa0(PCH_DB_a81fefa0), .PHI2(PHI2), .in_7(in_19),
    .ADH1(in_20), .ADH2(in_21), .ADH3(ADH3), .ADH4(in_23), .ADH5(in_24), .in_13(in_25), .in_14(in_26));
endmodule

module ABL_LOW_BIT (
  input  PHI1,
  input  PHI2,
  input  ADL_ABL_5bea59e2,
  input  L_0_ADLx_7ec67910,
  input  ADLx,
  output Ax
);

  wire and_1_out, and_2_out, not1_out, not_1_out;

  not not_1 (not_1_out, L_0_ADLx_7ec67910);
  and and_1 (and_1_out, not_1_out, ADLx);
  not not1 (not1_out, and_1_out);
  and and_2 (and_2_out, PHI1, ADL_ABL_5bea59e2);
  D_Flip_Flop #(.trigger("high")) not2_not3 (.D(not1_out), .clk(and_2_out), .Qn(Ax));  // open: Q, preset, reset

  // Notes on the sheet:
  //   not used
endmodule

module ABL_BIT (
  input  PHI1,
  input  PHI2,
  input  ADL_ABL_5bea59e2,
  input  ADLx,
  output Ax
);

  wire and_1_out, not1_out;

  and and_1 (and_1_out, PHI1, ADL_ABL_5bea59e2);
  not not1 (not1_out, ADLx);
  D_Flip_Flop #(.trigger("high")) not2_not3 (.D(not1_out), .clk(and_1_out), .Qn(Ax));  // open: Q, preset, reset

  // Notes on the sheet:
  //   not used
endmodule

module ABH_BIT (
  input  PHI1,
  input  PHI2,
  input  ADH_ABH_8f72aca9,
  input  ADHx,
  output Ax
);

  wire and_1_out, not1_out;

  and and_1 (and_1_out, PHI1, ADH_ABH_8f72aca9);
  not not1 (not1_out, ADHx);
  D_Flip_Flop #(.trigger("high")) not2_not3 (.D(not1_out), .clk(and_1_out), .Qn(Ax));  // open: Q, preset, reset

  // Notes on the sheet:
  //   not used
endmodule

module PCL_EVEN_BIT (
  input  PHI2,
  input  cin,
  input  ADL_PCL_9a95c372,
  input  PCL_PCL_4f350f4d,
  input  PCL_ADL_ee043dbc,
  input  PCL_DB_4172714e,
  input  ADLx_In,
  output DBx,
  output ADLx_Out,
  output cout,
  output sout,
  output PCL_Debug,
  output PCLS_Debug
);

  wire and_1_out, controlled_buffer_1_out, nand_1_out, not_1_out, PCL_qn;

  nor nor_1 (cout, cin, sout);
  assign controlled_buffer_1_out = PCL_PCL_4f350f4d ? PCL_Debug : 1'bz;  // Controlled_Buffer controlled_buffer_1
  assign controlled_buffer_1_out = ADL_PCL_9a95c372 ? ADLx_In : 1'bz;  // Controlled_Buffer controlled_buffer_2
  nand nand_1 (nand_1_out, cin, sout);
  not not_1 (not_1_out, cout);
  D_Flip_Flop #(.trigger("falling")) PCL (.D(and_1_out), .clk(PHI2), .Qn(PCL_qn));  // open: Q, preset, reset
  D_Flip_Flop #(.trigger("high")) PCLS (
    .D(controlled_buffer_1_out), .clk(1'b1), .Q(PCLS_Debug), .Qn(sout));  // open: preset, reset
  and and_1 (and_1_out, nand_1_out, not_1_out);
  not not_2 (PCL_Debug, PCL_qn);
  assign DBx = PCL_DB_4172714e ? PCL_Debug : 1'bz;  // Controlled_Buffer controlled_buffer_3
  assign ADLx_Out = PCL_ADL_ee043dbc ? PCL_Debug : 1'bz;  // Controlled_Buffer controlled_buffer_4

  // Notes on the sheet:
  //   posedge
endmodule

module PCL_ODD_BIT (
  input  PHI2,
  input  cin,
  input  ADL_PCL_9a95c372,
  input  PCL_PCL_4f350f4d,
  input  PCL_ADL_ee043dbc,
  input  PCL_DB_4172714e,
  input  ADLx_In,
  output DBx,
  output ADLx_Out,
  output cout,
  output sout,
  output PCL_Debug,
  output PCLS_Debug
);

  wire controlled_buffer_1_out, nor_1_out, not_1_out, not_2_out, not_3_out, or_1_out;

  nand nand_1 (cout, cin, not_1_out);
  not not_1 (not_1_out, sout);
  not not_2 (not_2_out, sout);
  not not_3 (not_3_out, cout);
  D_Flip_Flop #(.trigger("falling")) PCL (.D(or_1_out), .clk(PHI2), .Qn(PCL_Debug));  // open: Q, preset, reset
  assign controlled_buffer_1_out = PCL_PCL_4f350f4d ? PCL_Debug : 1'bz;  // Controlled_Buffer controlled_buffer_1
  D_Flip_Flop #(.trigger("high")) PCLS (
    .D(controlled_buffer_1_out), .clk(1'b1), .Q(PCLS_Debug), .Qn(sout));  // open: preset, reset
  assign controlled_buffer_1_out = ADL_PCL_9a95c372 ? ADLx_In : 1'bz;  // Controlled_Buffer controlled_buffer_2
  nor nor_1 (nor_1_out, cin, not_2_out);
  or or_1 (or_1_out, nor_1_out, not_3_out);
  assign DBx = PCL_DB_4172714e ? PCL_Debug : 1'bz;  // Controlled_Buffer controlled_buffer_3
  assign ADLx_Out = PCL_ADL_ee043dbc ? PCL_Debug : 1'bz;  // Controlled_Buffer controlled_buffer_4

  // Notes on the sheet:
  //   posedge
endmodule

module PCH_EVEN_BIT (
  input  PHI2,
  input  cin,
  input  ADH_PCH_61520abf,
  input  PCH_PCH_807b9fbd,
  input  PCH_ADH_ead93594,
  input  PCH_DB_a81fefa0,
  input  ADHx_In,
  output DBx,
  output ADHx_Out,
  output cout,
  output sout,
  output PCH_Debug,
  output PCHS_Debug
);

  wire controlled_buffer_1_out, nor_1_out, not_1_out, not_2_out, not_3_out, or_1_out;

  nand nand_1 (cout, cin, not_1_out);
  not not_1 (not_1_out, sout);
  not not_2 (not_2_out, sout);
  not not_3 (not_3_out, cout);
  D_Flip_Flop #(.trigger("falling")) PCH (.D(or_1_out), .clk(PHI2), .Qn(PCH_Debug));  // open: Q, preset, reset
  assign controlled_buffer_1_out = PCH_PCH_807b9fbd ? PCH_Debug : 1'bz;  // Controlled_Buffer controlled_buffer_1
  D_Flip_Flop #(.trigger("high")) PCHS (
    .D(controlled_buffer_1_out), .clk(1'b1), .Q(PCHS_Debug), .Qn(sout));  // open: preset, reset
  assign controlled_buffer_1_out = ADH_PCH_61520abf ? ADHx_In : 1'bz;  // Controlled_Buffer controlled_buffer_2
  nor nor_1 (nor_1_out, cin, not_2_out);
  or or_1 (or_1_out, nor_1_out, not_3_out);
  assign DBx = PCH_DB_a81fefa0 ? PCH_Debug : 1'bz;  // Controlled_Buffer controlled_buffer_3
  assign ADHx_Out = PCH_ADH_ead93594 ? PCH_Debug : 1'bz;  // Controlled_Buffer controlled_buffer_4

  // Notes on the sheet:
  //   posedge
endmodule

module PCH_ODD_BIT (
  input  PHI2,
  input  cin,
  input  ADH_PCH_61520abf,
  input  PCH_PCH_807b9fbd,
  input  PCH_ADH_ead93594,
  input  PCH_DB_a81fefa0,
  input  ADHx,
  output DBx,
  output out_9,
  output cout,
  output sout,
  output PCH_Debug,
  output PCHS_Debug
);

  wire and_1_out, controlled_buffer_1_out, nand_1_out, not_1_out, PCH_qn;

  nor nor_1 (cout, cin, sout);
  assign controlled_buffer_1_out = PCH_PCH_807b9fbd ? PCH_Debug : 1'bz;  // Controlled_Buffer controlled_buffer_1
  assign controlled_buffer_1_out = ADH_PCH_61520abf ? ADHx : 1'bz;  // Controlled_Buffer controlled_buffer_2
  nand nand_1 (nand_1_out, cin, sout);
  not not_1 (not_1_out, cout);
  D_Flip_Flop #(.trigger("falling")) PCH (.D(and_1_out), .clk(PHI2), .Qn(PCH_qn));  // open: Q, preset, reset
  D_Flip_Flop #(.trigger("high")) PCHS (
    .D(controlled_buffer_1_out), .clk(1'b1), .Q(PCHS_Debug), .Qn(sout));  // open: preset, reset
  and and_1 (and_1_out, nand_1_out, not_1_out);
  not not_2 (PCH_Debug, PCH_qn);
  assign DBx = PCH_DB_a81fefa0 ? PCH_Debug : 1'bz;  // Controlled_Buffer controlled_buffer_3
  assign out_9 = PCH_ADH_ead93594 ? PCH_Debug : 1'bz;  // Controlled_Buffer controlled_buffer_4

  // Notes on the sheet:
  //   posedge
endmodule

module PCL (
  input  PHI2,
  input  cin,
  input  ADL_PCL_9a95c372,
  input  PCL_PCL_4f350f4d,
  input  PCL_ADL_ee043dbc,
  input  PCL_DB_4172714e,
  input  in_7,
  input  in_8,
  input  ADL2,
  input  in_10,
  input  ADL4,
  input  in_12,
  input  ADL6,
  input  in_14,
  output ADL0,
  output ADL1,
  output out_17,
  output ADL3,
  output out_19,
  output ADL5,
  output out_21,
  output ADL7,
  output DB0,
  output DB1,
  output DB2,
  output DB3,
  output DB4,
  output DB5,
  output DB6,
  output DB7,
  output PCLC,
  output [7:0] PCL_Debug,
  output [7:0] PCLS_Debug
);

  wire _0_cout, _0_sout, _1_cout, _1_sout, _2_cout, _2_sout, _3_cout, _3_sout, _4_cout, _4_sout, _5_cout,
       _5_sout, _6_cout, _6_sout, _7_sout;

  PCL_EVEN_BIT _0 (
    .DBx(DB0), .ADLx_Out(ADL0), .cout(_0_cout), .sout(_0_sout), .PCL_Debug(PCL_Debug[0]),
    .PCLS_Debug(PCLS_Debug[0]), .cin(cin), .ADL_PCL_9a95c372(ADL_PCL_9a95c372),
    .PCL_PCL_4f350f4d(PCL_PCL_4f350f4d), .PCL_ADL_ee043dbc(PCL_ADL_ee043dbc),
    .PCL_DB_4172714e(PCL_DB_4172714e), .ADLx_In(in_7), .PHI2(PHI2));
  PCL_ODD_BIT _1 (
    .ADLx_Out(ADL1), .cout(_1_cout), .sout(_1_sout), .PCL_Debug(PCL_Debug[1]), .PCLS_Debug(PCLS_Debug[1]),
    .DBx(DB1), .cin(_0_cout), .ADL_PCL_9a95c372(ADL_PCL_9a95c372), .PCL_PCL_4f350f4d(PCL_PCL_4f350f4d),
    .PCL_ADL_ee043dbc(PCL_ADL_ee043dbc), .PCL_DB_4172714e(PCL_DB_4172714e), .ADLx_In(in_8), .PHI2(PHI2));
  PCL_EVEN_BIT _2 (
    .DBx(DB2), .ADLx_Out(out_17), .cout(_2_cout), .sout(_2_sout), .PCL_Debug(PCL_Debug[2]),
    .PCLS_Debug(PCLS_Debug[2]), .cin(_1_cout), .ADL_PCL_9a95c372(ADL_PCL_9a95c372),
    .PCL_PCL_4f350f4d(PCL_PCL_4f350f4d), .PCL_ADL_ee043dbc(PCL_ADL_ee043dbc),
    .PCL_DB_4172714e(PCL_DB_4172714e), .ADLx_In(ADL2), .PHI2(PHI2));
  PCL_ODD_BIT _3 (
    .ADLx_Out(ADL3), .cout(_3_cout), .sout(_3_sout), .PCL_Debug(PCL_Debug[3]), .PCLS_Debug(PCLS_Debug[3]),
    .DBx(DB3), .cin(_2_cout), .ADL_PCL_9a95c372(ADL_PCL_9a95c372), .PCL_PCL_4f350f4d(PCL_PCL_4f350f4d),
    .PCL_ADL_ee043dbc(PCL_ADL_ee043dbc), .PCL_DB_4172714e(PCL_DB_4172714e), .ADLx_In(in_10), .PHI2(PHI2));
  PCL_EVEN_BIT _4 (
    .DBx(DB4), .ADLx_Out(out_19), .cout(_4_cout), .sout(_4_sout), .PCL_Debug(PCL_Debug[4]),
    .PCLS_Debug(PCLS_Debug[4]), .cin(_3_cout), .ADL_PCL_9a95c372(ADL_PCL_9a95c372),
    .PCL_PCL_4f350f4d(PCL_PCL_4f350f4d), .PCL_ADL_ee043dbc(PCL_ADL_ee043dbc),
    .PCL_DB_4172714e(PCL_DB_4172714e), .ADLx_In(ADL4), .PHI2(PHI2));
  PCL_ODD_BIT _5 (
    .ADLx_Out(ADL5), .cout(_5_cout), .sout(_5_sout), .PCL_Debug(PCL_Debug[5]), .PCLS_Debug(PCLS_Debug[5]),
    .DBx(DB5), .cin(_4_cout), .ADL_PCL_9a95c372(ADL_PCL_9a95c372), .PCL_PCL_4f350f4d(PCL_PCL_4f350f4d),
    .PCL_ADL_ee043dbc(PCL_ADL_ee043dbc), .PCL_DB_4172714e(PCL_DB_4172714e), .ADLx_In(in_12), .PHI2(PHI2));
  PCL_EVEN_BIT _6 (
    .DBx(DB6), .ADLx_Out(out_21), .cout(_6_cout), .sout(_6_sout), .PCL_Debug(PCL_Debug[6]),
    .PCLS_Debug(PCLS_Debug[6]), .cin(_5_cout), .ADL_PCL_9a95c372(ADL_PCL_9a95c372),
    .PCL_PCL_4f350f4d(PCL_PCL_4f350f4d), .PCL_ADL_ee043dbc(PCL_ADL_ee043dbc),
    .PCL_DB_4172714e(PCL_DB_4172714e), .ADLx_In(ADL6), .PHI2(PHI2));
  PCL_ODD_BIT _7 (
    .ADLx_Out(ADL7), .sout(_7_sout), .PCL_Debug(PCL_Debug[7]), .PCLS_Debug(PCLS_Debug[7]), .DBx(DB7),
    .cin(_6_cout), .ADL_PCL_9a95c372(ADL_PCL_9a95c372), .PCL_PCL_4f350f4d(PCL_PCL_4f350f4d),
    .PCL_ADL_ee043dbc(PCL_ADL_ee043dbc), .PCL_DB_4172714e(PCL_DB_4172714e), .ADLx_In(in_14), .PHI2(PHI2));  // open: cout
  or or_1 (PCLC, _0_sout, _1_sout, _2_sout, _3_sout, _4_sout, _5_sout, _6_sout, _7_sout);
endmodule

module PCH (
  input  PHI2,
  input  cin,
  input  ADH_PCH_61520abf,
  input  PCH_PCH_807b9fbd,
  input  PCH_ADH_ead93594,
  input  PCH_DB_a81fefa0,
  input  in_7,
  input  ADH1,
  input  ADH2,
  input  ADH3,
  input  ADH4,
  input  ADH5,
  input  in_13,
  input  in_14,
  output ADH0,
  output out_16,
  output out_17,
  output out_18,
  output out_19,
  output out_20,
  output ADH6,
  output ADH7,
  output DB0,
  output DB1,
  output DB2,
  output DB3,
  output DB4,
  output DB5,
  output DB6,
  output DB7,
  output [7:0] PCH_Debug,
  output [7:0] PCHS_Debug
);

  wire _0_cout, _0_sout, _1_cout, _1_sout, _2_cout, _2_sout, _3_sout, not_1_out, or_1_out,
       pch_even_bit_1_cout, pch_odd_bit_1_cout, pch_odd_bit_2_cout;

  not not_1 (not_1_out, cin);
  PCH_EVEN_BIT _0 (
    .ADHx_Out(ADH0), .cout(_0_cout), .sout(_0_sout), .PCH_Debug(PCH_Debug[0]), .PCHS_Debug(PCHS_Debug[0]),
    .DBx(DB0), .cin(cin), .ADH_PCH_61520abf(ADH_PCH_61520abf), .PCH_PCH_807b9fbd(PCH_PCH_807b9fbd),
    .PCH_ADH_ead93594(PCH_ADH_ead93594), .PCH_DB_a81fefa0(PCH_DB_a81fefa0), .ADHx_In(in_7), .PHI2(PHI2));
  PCH_ODD_BIT _1 (
    .DBx(DB1), .out_9(out_16), .cout(_1_cout), .sout(_1_sout), .PCH_Debug(PCH_Debug[1]),
    .PCHS_Debug(PCHS_Debug[1]), .cin(_0_cout), .ADH_PCH_61520abf(ADH_PCH_61520abf),
    .PCH_PCH_807b9fbd(PCH_PCH_807b9fbd), .PCH_ADH_ead93594(PCH_ADH_ead93594),
    .PCH_DB_a81fefa0(PCH_DB_a81fefa0), .ADHx(ADH1), .PHI2(PHI2));
  PCH_EVEN_BIT _2 (
    .ADHx_Out(out_17), .cout(_2_cout), .sout(_2_sout), .PCH_Debug(PCH_Debug[2]), .PCHS_Debug(PCHS_Debug[2]),
    .DBx(DB2), .cin(_1_cout), .ADH_PCH_61520abf(ADH_PCH_61520abf), .PCH_PCH_807b9fbd(PCH_PCH_807b9fbd),
    .PCH_ADH_ead93594(PCH_ADH_ead93594), .PCH_DB_a81fefa0(PCH_DB_a81fefa0), .ADHx_In(ADH2), .PHI2(PHI2));
  PCH_ODD_BIT _3 (
    .DBx(DB3), .out_9(out_18), .sout(_3_sout), .PCH_Debug(PCH_Debug[3]), .PCHS_Debug(PCHS_Debug[3]),
    .cin(_2_cout), .ADH_PCH_61520abf(ADH_PCH_61520abf), .PCH_PCH_807b9fbd(PCH_PCH_807b9fbd),
    .PCH_ADH_ead93594(PCH_ADH_ead93594), .PCH_DB_a81fefa0(PCH_DB_a81fefa0), .ADHx(ADH3), .PHI2(PHI2));  // open: cout
  PCH_ODD_BIT pch_odd_bit_1 (
    .DBx(DB4), .out_9(out_19), .cout(pch_odd_bit_1_cout), .PCH_Debug(PCH_Debug[4]),
    .PCHS_Debug(PCHS_Debug[4]), .cin(or_1_out), .ADH_PCH_61520abf(ADH_PCH_61520abf),
    .PCH_PCH_807b9fbd(PCH_PCH_807b9fbd), .PCH_ADH_ead93594(PCH_ADH_ead93594),
    .PCH_DB_a81fefa0(PCH_DB_a81fefa0), .ADHx(ADH4), .PHI2(PHI2));  // open: sout
  PCH_EVEN_BIT pch_even_bit_1 (
    .ADHx_Out(out_20), .cout(pch_even_bit_1_cout), .PCH_Debug(PCH_Debug[5]), .PCHS_Debug(PCHS_Debug[5]),
    .DBx(DB5), .cin(pch_odd_bit_1_cout), .ADH_PCH_61520abf(ADH_PCH_61520abf),
    .PCH_PCH_807b9fbd(PCH_PCH_807b9fbd), .PCH_ADH_ead93594(PCH_ADH_ead93594),
    .PCH_DB_a81fefa0(PCH_DB_a81fefa0), .ADHx_In(ADH5), .PHI2(PHI2));  // open: sout
  PCH_ODD_BIT pch_odd_bit_2 (
    .DBx(DB6), .out_9(ADH6), .cout(pch_odd_bit_2_cout), .PCH_Debug(PCH_Debug[6]), .PCHS_Debug(PCHS_Debug[6]),
    .cin(pch_even_bit_1_cout), .ADH_PCH_61520abf(ADH_PCH_61520abf), .PCH_PCH_807b9fbd(PCH_PCH_807b9fbd),
    .PCH_ADH_ead93594(PCH_ADH_ead93594), .PCH_DB_a81fefa0(PCH_DB_a81fefa0), .ADHx(in_13), .PHI2(PHI2));  // open: sout
  PCH_EVEN_BIT _6 (
    .ADHx_Out(ADH7), .PCH_Debug(PCH_Debug[7]), .PCHS_Debug(PCHS_Debug[7]), .DBx(DB7),
    .cin(pch_odd_bit_2_cout), .ADH_PCH_61520abf(ADH_PCH_61520abf), .PCH_PCH_807b9fbd(PCH_PCH_807b9fbd),
    .PCH_ADH_ead93594(PCH_ADH_ead93594), .PCH_DB_a81fefa0(PCH_DB_a81fefa0), .ADHx_In(in_14), .PHI2(PHI2));  // open: cout, sout
  or or_1 (or_1_out, not_1_out, _0_sout, _1_sout, _2_sout, _3_sout);

  // Notes on the sheet:
  //   PCHC
endmodule

module ALU_OPS (
  input  NDB_ADD_ee0a1870,
  input  DB_ADD_48d85b7e,
  input  L_0_ADD_81d17e61,
  input  SB_ADD_0eab26ac,
  input  ADL_ADD_e28b8a30,
  input  ANDS,
  input  EORS,
  input  ORS,
  input  SRS,
  input  SUMS,
  input  L_cin_af3836dd,
  input  DC3,
  input  SB0,
  input  SB1,
  input  SB2,
  input  SB3,
  input  SB4,
  input  SB5,
  input  SB6,
  input  SB7,
  input  DB0,
  input  DB1,
  input  DB2,
  input  DB3,
  input  DB4,
  input  DB5,
  input  DB6,
  input  DB7,
  input  ADL0,
  input  ADL1,
  input  ADL2,
  input  ADL3,
  input  ADL4,
  input  ADL5,
  input  ADL6,
  input  ADL7,
  output L_carry3_9e435978,
  output carry4,
  output carry6,
  output L_carry7_b3181e70,
  output res0,
  output res1,
  output res2,
  output res3,
  output res4,
  output res5,
  output res6,
  output res7,
  output nor0,
  output nor1,
  output nor2,
  output nor3,
  output nor4,
  output nor5,
  output nor6,
  output nor7,
  output nand0,
  output nand1,
  output nand2,
  output nand3,
  output nand4,
  output nand5,
  output nand6,
  output nand7,
  output xor0,
  output xor1,
  output xor2,
  output xor3,
  output xor4,
  output xor5,
  output xor6,
  output xor7,
  output [7:0] AI_Debug,
  output [7:0] BI_Debug
);

  wire _0_cout, _1_l_cout_4dd9971a, _2_cout, _5_l_cout_4dd9971a, and_1_out, not_1_out;

  ALU_EVEN_BIT _0 (
    .AI_Debug(AI_Debug[0]), .BI_Debug(BI_Debug[0]), .L_res_da3ec8b2(res0), .cout(_0_cout), .\nor (nor0),
    .\nand (nand0), .\xor (xor0), .L_0_ADD_81d17e61(L_0_ADD_81d17e61), .SB_ADD_0eab26ac(SB_ADD_0eab26ac),
    .ADL_ADD_e28b8a30(ADL_ADD_e28b8a30), .ANDS(ANDS), .EORS(EORS), .ORS(ORS), .SRS(SRS), .SUMS(SUMS),
    .L_cin_af3836dd(L_cin_af3836dd), .prev_res(nand1), .SBx(SB0), .NDB_ADD_ee0a1870(NDB_ADD_ee0a1870),
    .DBx(DB0), .ADLx(ADL0), .DB_ADD_48d85b7e(DB_ADD_48d85b7e));
  ALU_ODD_BIT _1 (
    .AI_Debug(AI_Debug[1]), .BI_Debug(BI_Debug[1]), .L_res_da3ec8b2(res1),
    .L_cout_4dd9971a(_1_l_cout_4dd9971a), .\nor (nor1), .\nand (nand1), .\xor (xor1),
    .L_0_ADD_81d17e61(L_0_ADD_81d17e61), .SB_ADD_0eab26ac(SB_ADD_0eab26ac),
    .ADL_ADD_e28b8a30(ADL_ADD_e28b8a30), .ANDS(ANDS), .EORS(EORS), .ORS(ORS), .SRS(SRS), .SUMS(SUMS),
    .cin(_0_cout), .prev_res(nand2), .SBx(SB1), .NDB_ADD_ee0a1870(NDB_ADD_ee0a1870), .DBx(DB1), .ADLx(ADL1),
    .DB_ADD_48d85b7e(DB_ADD_48d85b7e));
  ALU_EVEN_BIT _2 (
    .AI_Debug(AI_Debug[2]), .BI_Debug(BI_Debug[2]), .L_res_da3ec8b2(res2), .cout(_2_cout), .\nor (nor2),
    .\nand (nand2), .\xor (xor2), .L_0_ADD_81d17e61(L_0_ADD_81d17e61), .SB_ADD_0eab26ac(SB_ADD_0eab26ac),
    .ADL_ADD_e28b8a30(ADL_ADD_e28b8a30), .ANDS(ANDS), .EORS(EORS), .ORS(ORS), .SRS(SRS), .SUMS(SUMS),
    .L_cin_af3836dd(_1_l_cout_4dd9971a), .prev_res(nand3), .SBx(SB2), .NDB_ADD_ee0a1870(NDB_ADD_ee0a1870),
    .DBx(DB2), .ADLx(ADL2), .DB_ADD_48d85b7e(DB_ADD_48d85b7e));
  ALU_ODD_BIT _3 (
    .AI_Debug(AI_Debug[3]), .BI_Debug(BI_Debug[3]), .L_res_da3ec8b2(res3),
    .L_cout_4dd9971a(L_carry3_9e435978), .\nor (nor3), .\nand (nand3), .\xor (xor3),
    .L_0_ADD_81d17e61(L_0_ADD_81d17e61), .SB_ADD_0eab26ac(SB_ADD_0eab26ac),
    .ADL_ADD_e28b8a30(ADL_ADD_e28b8a30), .ANDS(ANDS), .EORS(EORS), .ORS(ORS), .SRS(SRS), .SUMS(SUMS),
    .cin(_2_cout), .prev_res(nand4), .SBx(SB3), .NDB_ADD_ee0a1870(NDB_ADD_ee0a1870), .DBx(DB3), .ADLx(ADL3),
    .DB_ADD_48d85b7e(DB_ADD_48d85b7e));
  not not_1 (not_1_out, DC3);
  and and_1 (and_1_out, L_carry3_9e435978, not_1_out);
  ALU_EVEN_BIT _4 (
    .AI_Debug(AI_Debug[4]), .BI_Debug(BI_Debug[4]), .L_res_da3ec8b2(res4), .cout(carry4), .\nor (nor4),
    .\nand (nand4), .\xor (xor4), .L_0_ADD_81d17e61(L_0_ADD_81d17e61), .SB_ADD_0eab26ac(SB_ADD_0eab26ac),
    .ADL_ADD_e28b8a30(ADL_ADD_e28b8a30), .ANDS(ANDS), .EORS(EORS), .ORS(ORS), .SRS(SRS), .SUMS(SUMS),
    .L_cin_af3836dd(and_1_out), .prev_res(nand5), .SBx(SB4), .NDB_ADD_ee0a1870(NDB_ADD_ee0a1870), .DBx(DB4),
    .ADLx(ADL4), .DB_ADD_48d85b7e(DB_ADD_48d85b7e));
  ALU_ODD_BIT _5 (
    .AI_Debug(AI_Debug[5]), .BI_Debug(BI_Debug[5]), .L_res_da3ec8b2(res5),
    .L_cout_4dd9971a(_5_l_cout_4dd9971a), .\nor (nor5), .\nand (nand5), .\xor (xor5),
    .L_0_ADD_81d17e61(L_0_ADD_81d17e61), .SB_ADD_0eab26ac(SB_ADD_0eab26ac),
    .ADL_ADD_e28b8a30(ADL_ADD_e28b8a30), .ANDS(ANDS), .EORS(EORS), .ORS(ORS), .SRS(SRS), .SUMS(SUMS),
    .cin(carry4), .prev_res(nand6), .SBx(SB5), .NDB_ADD_ee0a1870(NDB_ADD_ee0a1870), .DBx(DB5), .ADLx(ADL5),
    .DB_ADD_48d85b7e(DB_ADD_48d85b7e));
  ALU_EVEN_BIT _6 (
    .AI_Debug(AI_Debug[6]), .BI_Debug(BI_Debug[6]), .L_res_da3ec8b2(res6), .cout(carry6), .\nor (nor6),
    .\nand (nand6), .\xor (xor6), .L_0_ADD_81d17e61(L_0_ADD_81d17e61), .SB_ADD_0eab26ac(SB_ADD_0eab26ac),
    .ADL_ADD_e28b8a30(ADL_ADD_e28b8a30), .ANDS(ANDS), .EORS(EORS), .ORS(ORS), .SRS(SRS), .SUMS(SUMS),
    .L_cin_af3836dd(_5_l_cout_4dd9971a), .prev_res(nand7), .SBx(SB6), .NDB_ADD_ee0a1870(NDB_ADD_ee0a1870),
    .DBx(DB6), .ADLx(ADL6), .DB_ADD_48d85b7e(DB_ADD_48d85b7e));
  ALU_ODD_BIT _7 (
    .AI_Debug(AI_Debug[7]), .BI_Debug(BI_Debug[7]), .L_res_da3ec8b2(res7),
    .L_cout_4dd9971a(L_carry7_b3181e70), .\nor (nor7), .\nand (nand7), .\xor (xor7),
    .L_0_ADD_81d17e61(L_0_ADD_81d17e61), .SB_ADD_0eab26ac(SB_ADD_0eab26ac),
    .ADL_ADD_e28b8a30(ADL_ADD_e28b8a30), .ANDS(ANDS), .EORS(EORS), .ORS(ORS), .SRS(SRS), .SUMS(SUMS),
    .cin(carry6), .prev_res(1'b1), .SBx(SB7), .NDB_ADD_ee0a1870(NDB_ADD_ee0a1870), .DBx(DB7), .ADLx(ADL7),
    .DB_ADD_48d85b7e(DB_ADD_48d85b7e));
endmodule

module ALU_EVEN_BIT (
  input  NDB_ADD_ee0a1870,
  input  DB_ADD_48d85b7e,
  input  L_0_ADD_81d17e61,
  input  SB_ADD_0eab26ac,
  input  ADL_ADD_e28b8a30,
  input  ANDS,
  input  EORS,
  input  ORS,
  input  SRS,
  input  SUMS,
  input  L_cin_af3836dd,
  input  prev_res,
  input  SBx,
  input  DBx,
  input  ADLx,
  output L_res_da3ec8b2,
  output cout,
  output AI_Debug,
  output \nor ,
  output \nand ,
  output BI_Debug,
  output \xor 
);

  wire and_1_out, controlled_buffer_1_out, controlled_buffer_3_out, nand_2_out, nand_3_out, nand_4_out,
       nor_2_out, not_1_out, not_2_out, not_3_out, not_4_out, not_5_out;

  not not_1 (not_1_out, DBx);
  assign controlled_buffer_1_out = L_0_ADD_81d17e61 ? 1'b0 : 1'bz;  // Controlled_Buffer controlled_buffer_1
  assign controlled_buffer_1_out = SB_ADD_0eab26ac ? SBx : 1'bz;  // Controlled_Buffer controlled_buffer_2
  assign controlled_buffer_3_out = DB_ADD_48d85b7e ? DBx : 1'bz;  // Controlled_Buffer controlled_buffer_3
  assign controlled_buffer_3_out = NDB_ADD_ee0a1870 ? not_1_out : 1'bz;  // Controlled_Buffer controlled_buffer_4
  assign controlled_buffer_3_out = ADL_ADD_e28b8a30 ? ADLx : 1'bz;  // Controlled_Buffer controlled_buffer_5
  D_Latch AI (.Q(AI_Debug), .D(controlled_buffer_1_out), .EN(1'b1));  // open: NOT_Q
  D_Latch BI (.Q(BI_Debug), .D(controlled_buffer_3_out), .EN(1'b1));  // open: NOT_Q
  not not_2 (not_2_out, \nor );
  not not_3 (not_3_out, L_cin_af3836dd);
  nand nand_1 (\nand , AI_Debug, BI_Debug);
  nor nor_1 (\nor , AI_Debug, BI_Debug);
  nand nand_2 (nand_2_out, not_2_out, \nand );
  nand nand_3 (nand_3_out, not_3_out, nand_2_out);
  not not_4 (not_4_out, nor_2_out);
  nor nor_2 (nor_2_out, not_3_out, nand_2_out);
  nand nand_4 (nand_4_out, L_cin_af3836dd, \nand );
  not not_5 (not_5_out, \nor );
  and and_1 (and_1_out, nand_3_out, not_4_out);
  and and_2 (cout, nand_4_out, not_5_out);
  assign L_res_da3ec8b2 = ANDS ? \nand  : 1'bz;  // Controlled_Buffer controlled_buffer_6
  assign L_res_da3ec8b2 = ORS ? \nor  : 1'bz;  // Controlled_Buffer controlled_buffer_7
  assign L_res_da3ec8b2 = EORS ? nand_2_out : 1'bz;  // Controlled_Buffer controlled_buffer_8
  assign L_res_da3ec8b2 = SRS ? prev_res : 1'bz;  // Controlled_Buffer controlled_buffer_9
  assign L_res_da3ec8b2 = SUMS ? and_1_out : 1'bz;  // Controlled_Buffer controlled_buffer_10
  not not_6 (\xor , nand_2_out);

  // Notes on the sheet:
  //   xnor
  //   xor
endmodule

module ALU_ODD_BIT (
  input  NDB_ADD_ee0a1870,
  input  DB_ADD_48d85b7e,
  input  L_0_ADD_81d17e61,
  input  SB_ADD_0eab26ac,
  input  ADL_ADD_e28b8a30,
  input  ANDS,
  input  EORS,
  input  ORS,
  input  SRS,
  input  SUMS,
  input  cin,
  input  prev_res,
  input  SBx,
  input  DBx,
  input  ADLx,
  output L_res_da3ec8b2,
  output L_cout_4dd9971a,
  output AI_Debug,
  output \nor ,
  output \nand ,
  output BI_Debug,
  output \xor 
);

  wire and_1_out, controlled_buffer_1_out, controlled_buffer_3_out, nand_2_out, nand_3_out, nor_3_out,
       not_1_out, not_2_out, not_3_out, not_4_out, not_5_out, not_6_out;

  not not_1 (not_1_out, DBx);
  assign controlled_buffer_1_out = L_0_ADD_81d17e61 ? 1'b0 : 1'bz;  // Controlled_Buffer controlled_buffer_1
  assign controlled_buffer_1_out = SB_ADD_0eab26ac ? SBx : 1'bz;  // Controlled_Buffer controlled_buffer_2
  assign controlled_buffer_3_out = DB_ADD_48d85b7e ? DBx : 1'bz;  // Controlled_Buffer controlled_buffer_3
  assign controlled_buffer_3_out = NDB_ADD_ee0a1870 ? not_1_out : 1'bz;  // Controlled_Buffer controlled_buffer_4
  assign controlled_buffer_3_out = ADL_ADD_e28b8a30 ? ADLx : 1'bz;  // Controlled_Buffer controlled_buffer_5
  D_Latch AI (.Q(AI_Debug), .D(controlled_buffer_1_out), .EN(1'b1));  // open: NOT_Q
  D_Latch BI (.Q(BI_Debug), .D(controlled_buffer_3_out), .EN(1'b1));  // open: NOT_Q
  not not_2 (not_2_out, \nand );
  not not_3 (not_3_out, cin);
  not not_4 (not_4_out, \nor );
  nand nand_1 (\nand , AI_Debug, BI_Debug);
  nor nor_1 (\nor , AI_Debug, BI_Debug);
  nor nor_2 (\xor , not_2_out, \nor );
  nand nand_2 (nand_2_out, not_3_out, \xor );
  not not_5 (not_5_out, nor_3_out);
  nor nor_3 (nor_3_out, not_3_out, \xor );
  nand nand_3 (nand_3_out, cin, not_4_out);
  not not_6 (not_6_out, not_2_out);
  and and_1 (and_1_out, nand_2_out, not_5_out);
  and and_2 (L_cout_4dd9971a, nand_3_out, not_6_out);
  assign L_res_da3ec8b2 = ANDS ? \nand  : 1'bz;  // Controlled_Buffer controlled_buffer_6
  assign L_res_da3ec8b2 = ORS ? \nor  : 1'bz;  // Controlled_Buffer controlled_buffer_7
  assign L_res_da3ec8b2 = EORS ? \xor  : 1'bz;  // Controlled_Buffer controlled_buffer_8
  assign L_res_da3ec8b2 = SRS ? prev_res : 1'bz;  // Controlled_Buffer controlled_buffer_9
  assign L_res_da3ec8b2 = SUMS ? and_1_out : 1'bz;  // Controlled_Buffer controlled_buffer_10

  // Notes on the sheet:
  //   xor
  //   xor
endmodule
module BCD_CARRY (
  input  L_ACIN_e173f520,
  input  carry4,
  input  L_DAA_82b80d94,
  input  [7:0] \nor ,
  input  [7:0] \nand ,
  input  [7:0] \xor ,
  output DC3,
  output DC7
);

  wire and_1_out, L_1_28cbbb7d_out, L_2_143403ae_out, L_3_39a566ac_out, L_4_1_c70c8704_out, nand_1_out,
       nand_2_out, nor_1_out, nor_2_out, nor_3_out, nor_4_out, nor_5_out, nor_6_out, not_1_out, not_2_out,
       not_3_out, not_4_out, not_5_out, not_6_out, not_7_out, not_8_out, not_9_out, or_1_out, or_2_out;

  nand nand_1 (nand_1_out, L_ACIN_e173f520, \nand [0]);
  not not_1 (not_1_out, \nor [0]);
  not not_2 (not_2_out, \nand [5]);
  not not_3 (not_3_out, \nand [2]);
  not not_4 (not_4_out, \nand [1]);
  and and_1 (and_1_out, nand_1_out, not_1_out);
  nor nor_1 (nor_1_out, not_3_out, \nor [2]);
  nor nor_2 (nor_2_out, and_1_out, nor_1_out, not_4_out, \xor [1]);
  not not_5 (not_5_out, \nand [1]);
  not not_6 (not_6_out, \nand [6]);
  nor L_4_1_c70c8704 (L_4_1_c70c8704_out, carry4, not_2_out, \xor [5], \xor [6]);
  nor nor_3 (nor_3_out, not_3_out, \xor [3]);
  nor nor_4 (nor_4_out, nor_3_out, nor_2_out);
  nor L_3_39a566ac (L_3_39a566ac_out, \nor [2], nand_2_out);
  nand nand_2 (nand_2_out, not_5_out, and_1_out);
  nor L_2_143403ae (L_2_143403ae_out, \xor [7], not_6_out);
  nor nor_5 (nor_5_out, L_2_143403ae_out, L_4_1_c70c8704_out);
  not not_7 (not_7_out, \xor [6]);
  nor nor_6 (nor_6_out, not_7_out, L_1_28cbbb7d_out);
  nand L_1_28cbbb7d (L_1_28cbbb7d_out, not_2_out, carry4);
  or or_1 (or_1_out, nor_4_out, L_3_39a566ac_out);
  or or_2 (or_2_out, nor_5_out, nor_6_out);
  and and_2 (DC3, or_1_out, not_8_out);
  not not_8 (not_8_out, L_DAA_82b80d94);
  and and_3 (DC7, or_2_out, not_9_out);
  not not_9 (not_9_out, L_DAA_82b80d94);

  // Notes on the sheet:
  //   c
  //   b
  //   ~(b | c)
  //   a
endmodule

module ALU_ADD (
  input  PHI2,
  input  ADD_SB06_a3738230,
  input  ADD_SB7_a8f4b77a,
  input  ADD_ADL_3fac4345,
  input  [7:0] L_res_da3ec8b2,
  output [7:0] L_ADDx_85db8c05,
  output SB0,
  output SB1,
  output SB2,
  output SB3,
  output SB4,
  output SB5,
  output SB6,
  output SB7,
  output ADL0,
  output ADL1,
  output ADL2,
  output ADL3,
  output ADL4,
  output ADL5,
  output ADL6,
  output ADL7,
  output [7:0] ADD_Debug
);

  D_Latch d_latch_1 (.Q(L_ADDx_85db8c05[0]), .NOT_Q(ADD_Debug[0]), .D(L_res_da3ec8b2[0]), .EN(PHI2));
  D_Latch d_latch_2 (.Q(L_ADDx_85db8c05[1]), .NOT_Q(ADD_Debug[1]), .D(L_res_da3ec8b2[1]), .EN(PHI2));
  D_Latch d_latch_3 (.Q(L_ADDx_85db8c05[2]), .NOT_Q(ADD_Debug[2]), .D(L_res_da3ec8b2[2]), .EN(PHI2));
  D_Latch d_latch_4 (.Q(L_ADDx_85db8c05[3]), .NOT_Q(ADD_Debug[3]), .D(L_res_da3ec8b2[3]), .EN(PHI2));
  D_Latch d_latch_5 (.Q(L_ADDx_85db8c05[4]), .NOT_Q(ADD_Debug[4]), .D(L_res_da3ec8b2[4]), .EN(PHI2));
  D_Latch d_latch_6 (.Q(L_ADDx_85db8c05[5]), .NOT_Q(ADD_Debug[5]), .D(L_res_da3ec8b2[5]), .EN(PHI2));
  D_Latch d_latch_7 (.Q(L_ADDx_85db8c05[6]), .NOT_Q(ADD_Debug[6]), .D(L_res_da3ec8b2[6]), .EN(PHI2));
  D_Latch d_latch_8 (.Q(L_ADDx_85db8c05[7]), .NOT_Q(ADD_Debug[7]), .D(L_res_da3ec8b2[7]), .EN(PHI2));
  assign SB0 = ADD_SB06_a3738230 ? ADD_Debug[0] : 1'bz;  // Controlled_Buffer controlled_buffer_1
  assign SB1 = ADD_SB06_a3738230 ? ADD_Debug[1] : 1'bz;  // Controlled_Buffer controlled_buffer_2
  assign SB2 = ADD_SB06_a3738230 ? ADD_Debug[2] : 1'bz;  // Controlled_Buffer controlled_buffer_3
  assign SB3 = ADD_SB06_a3738230 ? ADD_Debug[3] : 1'bz;  // Controlled_Buffer controlled_buffer_4
  assign SB4 = ADD_SB06_a3738230 ? ADD_Debug[4] : 1'bz;  // Controlled_Buffer controlled_buffer_5
  assign SB5 = ADD_SB06_a3738230 ? ADD_Debug[5] : 1'bz;  // Controlled_Buffer controlled_buffer_6
  assign SB6 = ADD_SB06_a3738230 ? ADD_Debug[6] : 1'bz;  // Controlled_Buffer controlled_buffer_7
  assign SB7 = ADD_SB7_a8f4b77a ? ADD_Debug[7] : 1'bz;  // Controlled_Buffer controlled_buffer_8
  assign ADL0 = ADD_ADL_3fac4345 ? ADD_Debug[0] : 1'bz;  // Controlled_Buffer controlled_buffer_9
  assign ADL1 = ADD_ADL_3fac4345 ? ADD_Debug[1] : 1'bz;  // Controlled_Buffer controlled_buffer_10
  assign ADL2 = ADD_ADL_3fac4345 ? ADD_Debug[2] : 1'bz;  // Controlled_Buffer controlled_buffer_11
  assign ADL3 = ADD_ADL_3fac4345 ? ADD_Debug[3] : 1'bz;  // Controlled_Buffer controlled_buffer_12
  assign ADL4 = ADD_ADL_3fac4345 ? ADD_Debug[4] : 1'bz;  // Controlled_Buffer controlled_buffer_13
  assign ADL5 = ADD_ADL_3fac4345 ? ADD_Debug[5] : 1'bz;  // Controlled_Buffer controlled_buffer_14
  assign ADL6 = ADD_ADL_3fac4345 ? ADD_Debug[6] : 1'bz;  // Controlled_Buffer controlled_buffer_15
  assign ADL7 = ADD_ADL_3fac4345 ? ADD_Debug[7] : 1'bz;  // Controlled_Buffer controlled_buffer_16
endmodule

module ALU_BCD (
  input  PHI2,
  input  L_carry3_9e435978,
  input  ACR,
  input  L_DAA_82b80d94,
  input  L_DSA_ea96e89b,
  input  SB0,
  input  SB1,
  input  SB2,
  input  SB3,
  input  SB4,
  input  SB5,
  input  SB6,
  input  SB7,
  input  [7:0] L_ADDx_85db8c05,
  output out0,
  output out1,
  output out2,
  output out3,
  output out4,
  output out5,
  output out6,
  output out7
);

  wire and_1_out, and_2_out, and_3_out, and_4_out, d_latch_1_not_q, d_latch_2_not_q, d_latch_3_q,
       d_latch_4_not_q, nand_1_out, nand_2_out, nand_3_out, nand_4_out, nand_5_out, nand_6_out, nand_7_out,
       nand_8_out, nand_9_out, nand_10_out, nand_11_out, nor_1_out, nor_2_out, nor_3_out, nor_4_out,
       nor_5_out, nor_6_out, nor_7_out, not_1_out, not_2_out, not_3_out, not_4_out, not_5_out, not_6_out,
       not_7_out, not_8_out, not_9_out, not_10_out, not_11_out, not_12_out;

  not not_1 (not_1_out, L_carry3_9e435978);
  not not_2 (not_2_out, L_DAA_82b80d94);
  nor nor_1 (nor_1_out, L_ADDx_85db8c05[1], L_ADDx_85db8c05[2]);
  not not_3 (not_3_out, nor_1_out);
  nand nand_1 (nand_1_out, L_ADDx_85db8c05[1], L_ADDx_85db8c05[2]);
  nand nand_2 (nand_2_out, L_ADDx_85db8c05[5], L_ADDx_85db8c05[6]);
  nor nor_2 (nor_2_out, L_ADDx_85db8c05[5], L_ADDx_85db8c05[6]);
  D_Latch d_latch_1 (.NOT_Q(d_latch_1_not_q), .D(nand_3_out), .EN(PHI2));  // open: Q
  nand nand_3 (nand_3_out, not_2_out, not_1_out);
  D_Latch d_latch_2 (.NOT_Q(d_latch_2_not_q), .D(not_2_out), .EN(PHI2));  // open: Q
  D_Latch d_latch_3 (.Q(d_latch_3_q), .D(nor_3_out), .EN(PHI2));  // open: NOT_Q
  nor nor_3 (nor_3_out, not_1_out, L_DSA_ea96e89b);
  D_Latch d_latch_4 (.NOT_Q(d_latch_4_not_q), .D(not_4_out), .EN(PHI2));  // open: Q
  not not_4 (not_4_out, L_DSA_ea96e89b);
  nand nand_4 (nand_4_out, L_ADDx_85db8c05[1], d_latch_1_not_q);
  nand nand_5 (nand_5_out, ~L_ADDx_85db8c05[1], d_latch_3_q);  // NAND_Gate
  nand nand_6 (nand_6_out, not_3_out, d_latch_3_q);
  nand nand_7 (nand_7_out, nand_1_out, d_latch_1_not_q);
  nand nand_8 (nand_8_out, L_ADDx_85db8c05[5], nor_4_out);
  nand nand_9 (nand_9_out, ~L_ADDx_85db8c05[5], nor_5_out);  // NAND_Gate
  nand nand_10 (nand_10_out, nand_2_out, nor_4_out);
  not not_5 (not_5_out, nor_2_out);
  nand nand_11 (nand_11_out, not_5_out, nor_5_out);
  not not_6 (not_6_out, ACR);
  and and_1 (and_1_out, nand_4_out, nand_5_out);
  and and_2 (and_2_out, nand_6_out, nand_7_out);
  and and_3 (and_3_out, nand_8_out, nand_9_out);
  and and_4 (and_4_out, nand_10_out, nand_11_out);
  nor nor_4 (nor_4_out, not_6_out, d_latch_2_not_q);
  nor nor_5 (nor_5_out, ACR, d_latch_4_not_q);
  nor nor_6 (nor_6_out, d_latch_3_q, d_latch_1_not_q);
  not not_7 (not_7_out, SB1);
  not not_8 (not_8_out, SB2);
  not not_9 (not_9_out, SB3);
  nor nor_7 (nor_7_out, nor_4_out, nor_5_out);
  not not_10 (not_10_out, SB5);
  not not_11 (not_11_out, SB6);
  not not_12 (not_12_out, SB7);
  xor xor_1 (out1, nor_6_out, not_7_out);
  xor xor_2 (out2, and_1_out, not_8_out);
  xor xor_3 (out3, and_2_out, not_9_out);
  xor xor_4 (out5, nor_7_out, not_10_out);
  xor xor_5 (out6, and_3_out, not_11_out);
  xor xor_6 (out7, and_4_out, not_12_out);

  assign out0 = SB0;
  assign out4 = SB4;

  // Notes on the sheet:
  //   DAAL
  //   DAAL
  //   DAAH
  //   DSAL
  //   DSAH
  //   DSAL
  //   DAAH
  //   DSAH
endmodule

module ALU_AC (
  input  PHI2,
  input  SB_AC_b159eec5,
  input  AC_SB_c49f602a,
  input  AC_DB_519ce409,
  input  SB_DB_641efa5a,
  input  SB_ADH_4f1456ff,
  input  L_0_ADH0_e340c71e,
  input  L_0_ADH17_f181a8fa,
  input  [7:0] ins,
  input  SB0,
  input  in_11,
  input  SB2,
  input  in_13,
  input  SB4,
  input  SB5,
  input  SB6,
  input  in_17,
  output [7:0] AC_Debug,
  output out_19,
  output SB1,
  output out_21,
  output SB3,
  output out_23,
  output out_24,
  output out_25,
  output SB7,
  output DB0,
  output DB1,
  output DB2,
  output DB3,
  output DB4,
  output DB5,
  output DB6,
  output DB7,
  output ADH0,
  output ADH1,
  output ADH2,
  output ADH3,
  output ADH4,
  output ADH5,
  output ADH6,
  output ADH7
);

  wire and_1_out, and_2_out, and_3_out, and_4_out, and_5_out, and_6_out, and_7_out, and_8_out,
       controlled_buffer_1_out, controlled_buffer_2_out, controlled_buffer_3_out, controlled_buffer_4_out,
       controlled_buffer_5_out, controlled_buffer_6_out, controlled_buffer_7_out, controlled_buffer_8_out;

  assign controlled_buffer_1_out = SB_AC_b159eec5 ? ins[0] : 1'bz;  // Controlled_Buffer controlled_buffer_1
  assign controlled_buffer_2_out = SB_AC_b159eec5 ? ins[1] : 1'bz;  // Controlled_Buffer controlled_buffer_2
  assign controlled_buffer_3_out = SB_AC_b159eec5 ? ins[2] : 1'bz;  // Controlled_Buffer controlled_buffer_3
  assign controlled_buffer_4_out = SB_AC_b159eec5 ? ins[3] : 1'bz;  // Controlled_Buffer controlled_buffer_4
  assign controlled_buffer_5_out = SB_AC_b159eec5 ? ins[4] : 1'bz;  // Controlled_Buffer controlled_buffer_5
  assign controlled_buffer_6_out = SB_AC_b159eec5 ? ins[5] : 1'bz;  // Controlled_Buffer controlled_buffer_6
  assign controlled_buffer_7_out = SB_AC_b159eec5 ? ins[6] : 1'bz;  // Controlled_Buffer controlled_buffer_7
  assign controlled_buffer_8_out = SB_AC_b159eec5 ? ins[7] : 1'bz;  // Controlled_Buffer controlled_buffer_8
  D_Latch d_latch_1 (.Q(AC_Debug[0]), .D(controlled_buffer_1_out), .EN(PHI2));  // open: NOT_Q
  D_Latch d_latch_2 (.Q(AC_Debug[1]), .D(controlled_buffer_2_out), .EN(PHI2));  // open: NOT_Q
  D_Latch d_latch_3 (.Q(AC_Debug[2]), .D(controlled_buffer_3_out), .EN(PHI2));  // open: NOT_Q
  D_Latch d_latch_4 (.Q(AC_Debug[3]), .D(controlled_buffer_4_out), .EN(PHI2));  // open: NOT_Q
  D_Latch d_latch_5 (.Q(AC_Debug[4]), .D(controlled_buffer_5_out), .EN(PHI2));  // open: NOT_Q
  D_Latch d_latch_6 (.Q(AC_Debug[5]), .D(controlled_buffer_6_out), .EN(PHI2));  // open: NOT_Q
  D_Latch d_latch_7 (.Q(AC_Debug[6]), .D(controlled_buffer_7_out), .EN(PHI2));  // open: NOT_Q
  D_Latch d_latch_8 (.Q(AC_Debug[7]), .D(controlled_buffer_8_out), .EN(PHI2));  // open: NOT_Q
  assign DB0 = SB_DB_641efa5a ? SB0 : 1'bz;  // Controlled_Buffer controlled_buffer_9
  assign DB1 = SB_DB_641efa5a ? in_11 : 1'bz;  // Controlled_Buffer controlled_buffer_10
  assign DB2 = SB_DB_641efa5a ? SB2 : 1'bz;  // Controlled_Buffer controlled_buffer_11
  assign DB3 = SB_DB_641efa5a ? in_13 : 1'bz;  // Controlled_Buffer controlled_buffer_12
  assign DB4 = SB_DB_641efa5a ? SB4 : 1'bz;  // Controlled_Buffer controlled_buffer_13
  assign DB5 = SB_DB_641efa5a ? SB5 : 1'bz;  // Controlled_Buffer controlled_buffer_14
  assign DB6 = SB_DB_641efa5a ? SB6 : 1'bz;  // Controlled_Buffer controlled_buffer_15
  assign DB7 = SB_DB_641efa5a ? in_17 : 1'bz;  // Controlled_Buffer controlled_buffer_16
  assign DB0 = AC_DB_519ce409 ? AC_Debug[0] : 1'bz;  // Controlled_Buffer controlled_buffer_17
  assign DB1 = AC_DB_519ce409 ? AC_Debug[1] : 1'bz;  // Controlled_Buffer controlled_buffer_18
  assign DB2 = AC_DB_519ce409 ? AC_Debug[2] : 1'bz;  // Controlled_Buffer controlled_buffer_19
  assign DB3 = AC_DB_519ce409 ? AC_Debug[3] : 1'bz;  // Controlled_Buffer controlled_buffer_20
  assign DB4 = AC_DB_519ce409 ? AC_Debug[4] : 1'bz;  // Controlled_Buffer controlled_buffer_21
  assign DB5 = AC_DB_519ce409 ? AC_Debug[5] : 1'bz;  // Controlled_Buffer controlled_buffer_22
  assign DB6 = AC_DB_519ce409 ? AC_Debug[6] : 1'bz;  // Controlled_Buffer controlled_buffer_23
  assign DB7 = AC_DB_519ce409 ? AC_Debug[7] : 1'bz;  // Controlled_Buffer controlled_buffer_24
  and and_1 (and_1_out, SB0, ~L_0_ADH0_e340c71e);  // AND_Gate
  and and_2 (and_2_out, in_11, ~L_0_ADH17_f181a8fa);  // AND_Gate
  and and_3 (and_3_out, SB2, ~L_0_ADH17_f181a8fa);  // AND_Gate
  and and_4 (and_4_out, in_13, ~L_0_ADH17_f181a8fa);  // AND_Gate
  and and_5 (and_5_out, SB4, ~L_0_ADH17_f181a8fa);  // AND_Gate
  and and_6 (and_6_out, SB5, ~L_0_ADH17_f181a8fa);  // AND_Gate
  and and_7 (and_7_out, SB6, ~L_0_ADH17_f181a8fa);  // AND_Gate
  and and_8 (and_8_out, in_17, ~L_0_ADH17_f181a8fa);  // AND_Gate
  assign out_19 = AC_SB_c49f602a ? AC_Debug[0] : 1'bz;  // Controlled_Buffer controlled_buffer_25
  assign SB1 = AC_SB_c49f602a ? AC_Debug[1] : 1'bz;  // Controlled_Buffer controlled_buffer_26
  assign out_21 = AC_SB_c49f602a ? AC_Debug[2] : 1'bz;  // Controlled_Buffer controlled_buffer_27
  assign SB3 = AC_SB_c49f602a ? AC_Debug[3] : 1'bz;  // Controlled_Buffer controlled_buffer_28
  assign out_23 = AC_SB_c49f602a ? AC_Debug[4] : 1'bz;  // Controlled_Buffer controlled_buffer_29
  assign out_24 = AC_SB_c49f602a ? AC_Debug[5] : 1'bz;  // Controlled_Buffer controlled_buffer_30
  assign out_25 = AC_SB_c49f602a ? AC_Debug[6] : 1'bz;  // Controlled_Buffer controlled_buffer_31
  assign SB7 = AC_SB_c49f602a ? AC_Debug[7] : 1'bz;  // Controlled_Buffer controlled_buffer_32
  assign ADH0 = SB_ADH_4f1456ff ? and_1_out : 1'bz;  // Controlled_Buffer controlled_buffer_33
  assign ADH1 = SB_ADH_4f1456ff ? and_2_out : 1'bz;  // Controlled_Buffer controlled_buffer_34
  assign ADH2 = SB_ADH_4f1456ff ? and_3_out : 1'bz;  // Controlled_Buffer controlled_buffer_35
  assign ADH3 = SB_ADH_4f1456ff ? and_4_out : 1'bz;  // Controlled_Buffer controlled_buffer_36
  assign ADH4 = SB_ADH_4f1456ff ? and_5_out : 1'bz;  // Controlled_Buffer controlled_buffer_37
  assign ADH5 = SB_ADH_4f1456ff ? and_6_out : 1'bz;  // Controlled_Buffer controlled_buffer_38
  assign ADH6 = SB_ADH_4f1456ff ? and_7_out : 1'bz;  // Controlled_Buffer controlled_buffer_39
  assign ADH7 = SB_ADH_4f1456ff ? and_8_out : 1'bz;  // Controlled_Buffer controlled_buffer_40
endmodule
