// Logisim project Lenghtcounterrev.circ as structural Verilog: 8 circuits, main circuit MAIN
module MAIN (
  input  W4003,
  input  W4015,
  input  nR4015,
  input  D0,
  input  D3,
  input  D4,
  input  D5,
  input  D6,
  input  D7,
  input  nLFO2,
  input  Halt,
  input  Res,
  output PHI1,
  output PHI2,
  output NOSQA,
  output D0_2
);

  wire clock_1_out, controlunit_1_step, counter_1_carry_out, masterclock_1_aclk, masterclock_1_naclk;
  wire [9:0] counter_2_q;

  Clock clock_1 (.out(clock_1_out));
  Masterclock masterclock_1 (
    .PHI0(clock_1_out), .RES(Res), .PHI1(PHI1), .PHI2(PHI2), .ACLK(masterclock_1_aclk),
    .nACLK(masterclock_1_naclk));
  Counter counter_1 (
    .nACLK(masterclock_1_naclk), .STEP(controlunit_1_step), .W4003(W4003), .D3(D3), .D4(D4), .D5(D5),
    .D6(D6), .D7(D7), .HALT(Halt), .RES(Res), .Carry_Out(counter_1_carry_out));
  ControlUnit controlunit_1 (
    .ACLK(masterclock_1_aclk), .nACLK(masterclock_1_naclk), .W4003(W4003), .Carry_In(counter_1_carry_out),
    .W4015(W4015), .D0(D0), .Res(Res), .nLFO2(nLFO2), .nR4015(nR4015), .NOSQA(NOSQA), .D0_2(D0_2),
    .STEP(controlunit_1_step));
  Counter_part #(.width(10), .max('h3ff), .trigger("falling")) counter_2 (
    .Q(counter_2_q), .clk(nLFO2), .clr(NOSQA));  // open: load, D, count, carry
  Register #(.width(10)) register_1 (.D(counter_2_q), .clk(NOSQA));  // open: en, Q, clr
endmodule

module Decoder (
  input  D3,
  input  D4,
  input  D5,
  input  D6,
  input  D7,
  output LC0,
  output LC1,
  output LC2,
  output LC3,
  output LC4,
  output LC5,
  output LC6,
  output LC7
);

  wire not_1_out, not_2_out, not_3_out, not_4_out, not_5_out, transistor_138_out, transistor_139_out,
       transistor_140_out, transistor_141_out, transistor_142_out, transistor_143_out, transistor_144_out,
       transistor_145_out, transistor_146_out, transistor_147_out, transistor_148_out, transistor_149_out,
       transistor_150_out, transistor_151_out, transistor_152_out, transistor_153_out, transistor_162_out,
       transistor_164_out, transistor_165_out, transistor_167_out, transistor_168_out, transistor_170_out,
       transistor_171_out, transistor_173_out, transistor_174_out, transistor_176_out, transistor_177_out,
       transistor_179_out, transistor_180_out, transistor_182_out, transistor_183_out, transistor_185_out;

  Pull_Resistor #(.pull(1)) pull_resistor_1 (.node(LC0));
  Transistor #(.\type ("n")) transistor_1 (.in(1'b0), .out(LC1), .gate(transistor_138_out));
  Transistor #(.\type ("n")) transistor_2 (.in(1'b0), .out(LC1), .gate(transistor_140_out));
  Transistor #(.\type ("n")) transistor_3 (.in(1'b0), .out(LC1), .gate(transistor_142_out));
  Transistor #(.\type ("n")) transistor_4 (.in(1'b0), .out(LC1), .gate(transistor_144_out));
  Transistor #(.\type ("n")) transistor_5 (.in(1'b0), .out(LC1), .gate(transistor_146_out));
  Transistor #(.\type ("n")) transistor_6 (.in(1'b0), .out(LC1), .gate(transistor_148_out));
  Transistor #(.\type ("n")) transistor_7 (.in(1'b0), .out(LC1), .gate(transistor_150_out));
  Transistor #(.\type ("n")) transistor_8 (.in(1'b0), .out(LC1), .gate(transistor_152_out));
  Transistor #(.\type ("n")) transistor_9 (.in(1'b0), .out(LC1), .gate(transistor_153_out));
  Transistor #(.\type ("n")) transistor_10 (.in(1'b0), .out(LC1), .gate(transistor_174_out));
  Transistor #(.\type ("n")) transistor_11 (.in(1'b0), .out(LC1), .gate(transistor_176_out));
  Transistor #(.\type ("n")) transistor_12 (.in(1'b0), .out(LC1), .gate(transistor_185_out));
  Pull_Resistor #(.pull(1)) pull_resistor_2 (.node(LC1));
  Transistor #(.\type ("n")) transistor_13 (.in(1'b0), .out(LC2), .gate(transistor_139_out));
  Transistor #(.\type ("n")) transistor_14 (.in(1'b0), .out(LC2), .gate(transistor_140_out));
  Transistor #(.\type ("n")) transistor_15 (.in(1'b0), .out(LC2), .gate(transistor_143_out));
  Transistor #(.\type ("n")) transistor_16 (.in(1'b0), .out(LC2), .gate(transistor_144_out));
  Transistor #(.\type ("n")) transistor_17 (.in(1'b0), .out(LC2), .gate(transistor_147_out));
  Transistor #(.\type ("n")) transistor_18 (.in(1'b0), .out(LC2), .gate(transistor_148_out));
  Transistor #(.\type ("n")) transistor_19 (.in(1'b0), .out(LC2), .gate(transistor_151_out));
  Transistor #(.\type ("n")) transistor_20 (.in(1'b0), .out(LC2), .gate(transistor_152_out));
  Transistor #(.\type ("n")) transistor_21 (.in(1'b0), .out(LC2), .gate(transistor_173_out));
  Transistor #(.\type ("n")) transistor_22 (.in(1'b0), .out(LC2), .gate(transistor_174_out));
  Transistor #(.\type ("n")) transistor_23 (.in(1'b0), .out(LC2), .gate(transistor_177_out));
  Transistor #(.\type ("n")) transistor_24 (.in(1'b0), .out(LC2), .gate(transistor_183_out));
  Transistor #(.\type ("n")) transistor_25 (.in(1'b0), .out(LC2), .gate(transistor_185_out));
  Pull_Resistor #(.pull(1)) pull_resistor_3 (.node(LC2));
  Transistor #(.\type ("n")) transistor_26 (.in(1'b0), .out(LC3), .gate(transistor_141_out));
  Transistor #(.\type ("n")) transistor_27 (.in(1'b0), .out(LC3), .gate(transistor_142_out));
  Transistor #(.\type ("n")) transistor_28 (.in(1'b0), .out(LC3), .gate(transistor_143_out));
  Transistor #(.\type ("n")) transistor_29 (.in(1'b0), .out(LC3), .gate(transistor_144_out));
  Transistor #(.\type ("n")) transistor_30 (.in(1'b0), .out(LC3), .gate(transistor_149_out));
  Transistor #(.\type ("n")) transistor_31 (.in(1'b0), .out(LC3), .gate(transistor_150_out));
  Transistor #(.\type ("n")) transistor_32 (.in(1'b0), .out(LC3), .gate(transistor_151_out));
  Transistor #(.\type ("n")) transistor_33 (.in(1'b0), .out(LC3), .gate(transistor_152_out));
  Transistor #(.\type ("n")) transistor_34 (.in(1'b0), .out(LC3), .gate(transistor_165_out));
  Transistor #(.\type ("n")) transistor_35 (.in(1'b0), .out(LC3), .gate(transistor_171_out));
  Transistor #(.\type ("n")) transistor_36 (.in(1'b0), .out(LC3), .gate(transistor_182_out));
  Transistor #(.\type ("n")) transistor_37 (.in(1'b0), .out(LC3), .gate(transistor_183_out));
  Pull_Resistor #(.pull(1)) pull_resistor_4 (.node(LC3));
  Transistor #(.\type ("n")) transistor_38 (.in(1'b0), .out(LC4), .gate(transistor_145_out));
  Transistor #(.\type ("n")) transistor_39 (.in(1'b0), .out(LC4), .gate(transistor_146_out));
  Transistor #(.\type ("n")) transistor_40 (.in(1'b0), .out(LC4), .gate(transistor_147_out));
  Transistor #(.\type ("n")) transistor_41 (.in(1'b0), .out(LC4), .gate(transistor_148_out));
  Transistor #(.\type ("n")) transistor_42 (.in(1'b0), .out(LC4), .gate(transistor_149_out));
  Transistor #(.\type ("n")) transistor_43 (.in(1'b0), .out(LC4), .gate(transistor_150_out));
  Transistor #(.\type ("n")) transistor_44 (.in(1'b0), .out(LC4), .gate(transistor_151_out));
  Transistor #(.\type ("n")) transistor_45 (.in(1'b0), .out(LC4), .gate(transistor_152_out));
  Transistor #(.\type ("n")) transistor_46 (.in(1'b0), .out(LC4), .gate(transistor_164_out));
  Transistor #(.\type ("n")) transistor_47 (.in(1'b0), .out(LC4), .gate(transistor_165_out));
  Transistor #(.\type ("n")) transistor_48 (.in(1'b0), .out(LC4), .gate(transistor_170_out));
  Transistor #(.\type ("n")) transistor_49 (.in(1'b0), .out(LC4), .gate(transistor_173_out));
  Transistor #(.\type ("n")) transistor_50 (.in(1'b0), .out(LC4), .gate(transistor_176_out));
  Transistor #(.\type ("n")) transistor_51 (.in(1'b0), .out(LC4), .gate(transistor_180_out));
  Transistor #(.\type ("n")) transistor_52 (.in(1'b0), .out(LC4), .gate(transistor_182_out));
  Transistor #(.\type ("n")) transistor_53 (.in(1'b0), .out(LC4), .gate(transistor_185_out));
  Pull_Resistor #(.pull(1)) pull_resistor_5 (.node(LC4));
  Transistor #(.\type ("n")) transistor_54 (.in(1'b0), .out(LC5), .gate(transistor_138_out));
  Transistor #(.\type ("n")) transistor_55 (.in(1'b0), .out(LC5), .gate(transistor_139_out));
  Transistor #(.\type ("n")) transistor_56 (.in(1'b0), .out(LC5), .gate(transistor_140_out));
  Transistor #(.\type ("n")) transistor_57 (.in(1'b0), .out(LC5), .gate(transistor_141_out));
  Transistor #(.\type ("n")) transistor_58 (.in(1'b0), .out(LC5), .gate(transistor_142_out));
  Transistor #(.\type ("n")) transistor_59 (.in(1'b0), .out(LC5), .gate(transistor_143_out));
  Transistor #(.\type ("n")) transistor_60 (.in(1'b0), .out(LC5), .gate(transistor_144_out));
  Transistor #(.\type ("n")) transistor_61 (.in(1'b0), .out(LC5), .gate(transistor_145_out));
  Transistor #(.\type ("n")) transistor_62 (.in(1'b0), .out(LC5), .gate(transistor_146_out));
  Transistor #(.\type ("n")) transistor_63 (.in(1'b0), .out(LC5), .gate(transistor_147_out));
  Transistor #(.\type ("n")) transistor_64 (.in(1'b0), .out(LC5), .gate(transistor_148_out));
  Transistor #(.\type ("n")) transistor_65 (.in(1'b0), .out(LC5), .gate(transistor_149_out));
  Transistor #(.\type ("n")) transistor_66 (.in(1'b0), .out(LC5), .gate(transistor_150_out));
  Transistor #(.\type ("n")) transistor_67 (.in(1'b0), .out(LC5), .gate(transistor_151_out));
  Transistor #(.\type ("n")) transistor_68 (.in(1'b0), .out(LC5), .gate(transistor_152_out));
  Transistor #(.\type ("n")) transistor_69 (.in(1'b0), .out(LC5), .gate(transistor_162_out));
  Transistor #(.\type ("n")) transistor_70 (.in(1'b0), .out(LC5), .gate(transistor_164_out));
  Transistor #(.\type ("n")) transistor_71 (.in(1'b0), .out(LC5), .gate(transistor_165_out));
  Transistor #(.\type ("n")) transistor_72 (.in(1'b0), .out(LC5), .gate(transistor_168_out));
  Transistor #(.\type ("n")) transistor_73 (.in(1'b0), .out(LC5), .gate(transistor_171_out));
  Transistor #(.\type ("n")) transistor_74 (.in(1'b0), .out(LC5), .gate(transistor_173_out));
  Transistor #(.\type ("n")) transistor_75 (.in(1'b0), .out(LC5), .gate(transistor_174_out));
  Transistor #(.\type ("n")) transistor_76 (.in(1'b0), .out(LC5), .gate(transistor_176_out));
  Transistor #(.\type ("n")) transistor_77 (.in(1'b0), .out(LC5), .gate(transistor_179_out));
  Transistor #(.\type ("n")) transistor_78 (.in(1'b0), .out(LC5), .gate(transistor_180_out));
  Transistor #(.\type ("n")) transistor_79 (.in(1'b0), .out(LC5), .gate(transistor_183_out));
  Transistor #(.\type ("n")) transistor_80 (.in(1'b0), .out(LC5), .gate(transistor_185_out));
  Pull_Resistor #(.pull(1)) pull_resistor_6 (.node(LC5));
  Transistor #(.\type ("n")) transistor_81 (.in(1'b0), .out(LC6), .gate(transistor_138_out));
  Transistor #(.\type ("n")) transistor_82 (.in(1'b0), .out(LC6), .gate(transistor_139_out));
  Transistor #(.\type ("n")) transistor_83 (.in(1'b0), .out(LC6), .gate(transistor_140_out));
  Transistor #(.\type ("n")) transistor_84 (.in(1'b0), .out(LC6), .gate(transistor_141_out));
  Transistor #(.\type ("n")) transistor_85 (.in(1'b0), .out(LC6), .gate(transistor_142_out));
  Transistor #(.\type ("n")) transistor_86 (.in(1'b0), .out(LC6), .gate(transistor_143_out));
  Transistor #(.\type ("n")) transistor_87 (.in(1'b0), .out(LC6), .gate(transistor_144_out));
  Transistor #(.\type ("n")) transistor_88 (.in(1'b0), .out(LC6), .gate(transistor_145_out));
  Transistor #(.\type ("n")) transistor_89 (.in(1'b0), .out(LC6), .gate(transistor_146_out));
  Transistor #(.\type ("n")) transistor_90 (.in(1'b0), .out(LC6), .gate(transistor_147_out));
  Transistor #(.\type ("n")) transistor_91 (.in(1'b0), .out(LC6), .gate(transistor_148_out));
  Transistor #(.\type ("n")) transistor_92 (.in(1'b0), .out(LC6), .gate(transistor_149_out));
  Transistor #(.\type ("n")) transistor_93 (.in(1'b0), .out(LC6), .gate(transistor_150_out));
  Transistor #(.\type ("n")) transistor_94 (.in(1'b0), .out(LC6), .gate(transistor_151_out));
  Transistor #(.\type ("n")) transistor_95 (.in(1'b0), .out(LC6), .gate(transistor_152_out));
  Transistor #(.\type ("n")) transistor_96 (.in(1'b0), .out(LC6), .gate(transistor_162_out));
  Transistor #(.\type ("n")) transistor_97 (.in(1'b0), .out(LC6), .gate(transistor_164_out));
  Transistor #(.\type ("n")) transistor_98 (.in(1'b0), .out(LC6), .gate(transistor_167_out));
  Transistor #(.\type ("n")) transistor_99 (.in(1'b0), .out(LC6), .gate(transistor_170_out));
  Transistor #(.\type ("n")) transistor_100 (.in(1'b0), .out(LC6), .gate(transistor_171_out));
  Transistor #(.\type ("n")) transistor_101 (.in(1'b0), .out(LC6), .gate(transistor_173_out));
  Transistor #(.\type ("n")) transistor_102 (.in(1'b0), .out(LC6), .gate(transistor_174_out));
  Transistor #(.\type ("n")) transistor_103 (.in(1'b0), .out(LC6), .gate(transistor_176_out));
  Transistor #(.\type ("n")) transistor_104 (.in(1'b0), .out(LC6), .gate(transistor_177_out));
  Transistor #(.\type ("n")) transistor_105 (.in(1'b0), .out(LC6), .gate(transistor_179_out));
  Transistor #(.\type ("n")) transistor_106 (.in(1'b0), .out(LC6), .gate(transistor_182_out));
  Transistor #(.\type ("n")) transistor_107 (.in(1'b0), .out(LC6), .gate(transistor_183_out));
  Transistor #(.\type ("n")) transistor_108 (.in(1'b0), .out(LC6), .gate(transistor_185_out));
  Pull_Resistor #(.pull(1)) pull_resistor_7 (.node(LC6));
  Transistor #(.\type ("n")) transistor_109 (.in(1'b0), .out(LC7), .gate(transistor_138_out));
  Transistor #(.\type ("n")) transistor_110 (.in(1'b0), .out(LC7), .gate(transistor_139_out));
  Transistor #(.\type ("n")) transistor_111 (.in(1'b0), .out(LC7), .gate(transistor_140_out));
  Transistor #(.\type ("n")) transistor_112 (.in(1'b0), .out(LC7), .gate(transistor_141_out));
  Transistor #(.\type ("n")) transistor_113 (.in(1'b0), .out(LC7), .gate(transistor_142_out));
  Transistor #(.\type ("n")) transistor_114 (.in(1'b0), .out(LC7), .gate(transistor_143_out));
  Transistor #(.\type ("n")) transistor_115 (.in(1'b0), .out(LC7), .gate(transistor_144_out));
  Transistor #(.\type ("n")) transistor_116 (.in(1'b0), .out(LC7), .gate(transistor_145_out));
  Transistor #(.\type ("n")) transistor_117 (.in(1'b0), .out(LC7), .gate(transistor_146_out));
  Transistor #(.\type ("n")) transistor_118 (.in(1'b0), .out(LC7), .gate(transistor_147_out));
  Transistor #(.\type ("n")) transistor_119 (.in(1'b0), .out(LC7), .gate(transistor_148_out));
  Transistor #(.\type ("n")) transistor_120 (.in(1'b0), .out(LC7), .gate(transistor_149_out));
  Transistor #(.\type ("n")) transistor_121 (.in(1'b0), .out(LC7), .gate(transistor_150_out));
  Transistor #(.\type ("n")) transistor_122 (.in(1'b0), .out(LC7), .gate(transistor_151_out));
  Transistor #(.\type ("n")) transistor_123 (.in(1'b0), .out(LC7), .gate(transistor_152_out));
  Transistor #(.\type ("n")) transistor_124 (.in(1'b0), .out(LC7), .gate(transistor_162_out));
  Transistor #(.\type ("n")) transistor_125 (.in(1'b0), .out(LC7), .gate(transistor_164_out));
  Transistor #(.\type ("n")) transistor_126 (.in(1'b0), .out(LC7), .gate(transistor_165_out));
  Transistor #(.\type ("n")) transistor_127 (.in(1'b0), .out(LC7), .gate(transistor_168_out));
  Transistor #(.\type ("n")) transistor_128 (.in(1'b0), .out(LC7), .gate(transistor_170_out));
  Transistor #(.\type ("n")) transistor_129 (.in(1'b0), .out(LC7), .gate(transistor_171_out));
  Transistor #(.\type ("n")) transistor_130 (.in(1'b0), .out(LC7), .gate(transistor_173_out));
  Transistor #(.\type ("n")) transistor_131 (.in(1'b0), .out(LC7), .gate(transistor_174_out));
  Transistor #(.\type ("n")) transistor_132 (.in(1'b0), .out(LC7), .gate(transistor_176_out));
  Transistor #(.\type ("n")) transistor_133 (.in(1'b0), .out(LC7), .gate(transistor_177_out));
  Transistor #(.\type ("n")) transistor_134 (.in(1'b0), .out(LC7), .gate(transistor_180_out));
  Transistor #(.\type ("n")) transistor_135 (.in(1'b0), .out(LC7), .gate(transistor_182_out));
  Transistor #(.\type ("n")) transistor_136 (.in(1'b0), .out(LC7), .gate(transistor_183_out));
  Transistor #(.\type ("n")) transistor_137 (.in(1'b0), .out(LC7), .gate(transistor_185_out));
  Pull_Resistor #(.pull(1)) pull_resistor_8 (.node(LC7));
  not not_1 (not_1_out, D3);
  Transistor #(.\type ("n"), .gate("br")) transistor_138 (.in(1'b0), .out(transistor_138_out), .gate(not_1_out));
  Transistor #(.\type ("n"), .gate("br")) transistor_139 (.in(1'b0), .out(transistor_139_out), .gate(not_1_out));
  Transistor #(.\type ("n"), .gate("br")) transistor_140 (.in(1'b0), .out(transistor_140_out), .gate(not_1_out));
  Transistor #(.\type ("n"), .gate("br")) transistor_141 (.in(1'b0), .out(transistor_141_out), .gate(not_1_out));
  Transistor #(.\type ("n"), .gate("br")) transistor_142 (.in(1'b0), .out(transistor_142_out), .gate(not_1_out));
  Transistor #(.\type ("n"), .gate("br")) transistor_143 (.in(1'b0), .out(transistor_143_out), .gate(not_1_out));
  Transistor #(.\type ("n"), .gate("br")) transistor_144 (.in(1'b0), .out(transistor_144_out), .gate(not_1_out));
  Transistor #(.\type ("n"), .gate("br")) transistor_145 (.in(1'b0), .out(transistor_145_out), .gate(not_1_out));
  Transistor #(.\type ("n"), .gate("br")) transistor_146 (.in(1'b0), .out(transistor_146_out), .gate(not_1_out));
  Transistor #(.\type ("n"), .gate("br")) transistor_147 (.in(1'b0), .out(transistor_147_out), .gate(not_1_out));
  Transistor #(.\type ("n"), .gate("br")) transistor_148 (.in(1'b0), .out(transistor_148_out), .gate(not_1_out));
  Transistor #(.\type ("n"), .gate("br")) transistor_149 (.in(1'b0), .out(transistor_149_out), .gate(not_1_out));
  Transistor #(.\type ("n"), .gate("br")) transistor_150 (.in(1'b0), .out(transistor_150_out), .gate(not_1_out));
  Transistor #(.\type ("n"), .gate("br")) transistor_151 (.in(1'b0), .out(transistor_151_out), .gate(not_1_out));
  Transistor #(.\type ("n"), .gate("br")) transistor_152 (.in(1'b0), .out(transistor_152_out), .gate(not_1_out));
  Transistor #(.\type ("n"), .gate("br")) transistor_153 (.in(1'b0), .out(transistor_153_out), .gate(not_1_out));
  Transistor #(.\type ("n"), .gate("br")) transistor_154 (.in(1'b0), .out(transistor_138_out), .gate(not_2_out));
  Transistor #(.\type ("n"), .gate("br")) transistor_155 (.in(1'b0), .out(transistor_140_out), .gate(not_2_out));
  Transistor #(.\type ("n"), .gate("br")) transistor_156 (.in(1'b0), .out(transistor_142_out), .gate(not_2_out));
  Transistor #(.\type ("n"), .gate("br")) transistor_157 (.in(1'b0), .out(transistor_144_out), .gate(not_2_out));
  Transistor #(.\type ("n"), .gate("br")) transistor_158 (.in(1'b0), .out(transistor_146_out), .gate(not_2_out));
  Transistor #(.\type ("n"), .gate("br")) transistor_159 (.in(1'b0), .out(transistor_148_out), .gate(not_2_out));
  Transistor #(.\type ("n"), .gate("br")) transistor_160 (.in(1'b0), .out(transistor_150_out), .gate(not_2_out));
  Transistor #(.\type ("n"), .gate("br")) transistor_161 (.in(1'b0), .out(transistor_152_out), .gate(not_2_out));
  Transistor #(.\type ("n"), .gate("br")) transistor_162 (.in(1'b0), .out(transistor_162_out), .gate(D3));
  Transistor #(.\type ("n"), .gate("br")) transistor_163 (.in(1'b0), .out(transistor_162_out), .gate(not_2_out));
  Transistor #(.\type ("n"), .gate("br")) transistor_164 (.in(1'b0), .out(transistor_164_out), .gate(D3));
  Transistor #(.\type ("n"), .gate("br")) transistor_165 (.in(1'b0), .out(transistor_165_out), .gate(D3));
  Transistor #(.\type ("n"), .gate("br")) transistor_166 (.in(1'b0), .out(transistor_165_out), .gate(not_2_out));
  Transistor #(.\type ("n"), .gate("br")) transistor_167 (.in(1'b0), .out(transistor_167_out), .gate(D3));
  Transistor #(.\type ("n"), .gate("br")) transistor_168 (.in(1'b0), .out(transistor_168_out), .gate(D3));
  Transistor #(.\type ("n"), .gate("br")) transistor_169 (.in(1'b0), .out(transistor_168_out), .gate(not_2_out));
  Transistor #(.\type ("n"), .gate("br")) transistor_170 (.in(1'b0), .out(transistor_170_out), .gate(D3));
  Transistor #(.\type ("n"), .gate("br")) transistor_171 (.in(1'b0), .out(transistor_171_out), .gate(D3));
  Transistor #(.\type ("n"), .gate("br")) transistor_172 (.in(1'b0), .out(transistor_171_out), .gate(not_2_out));
  Transistor #(.\type ("n"), .gate("br")) transistor_173 (.in(1'b0), .out(transistor_173_out), .gate(D3));
  Transistor #(.\type ("n"), .gate("br")) transistor_174 (.in(1'b0), .out(transistor_174_out), .gate(not_2_out));
  Transistor #(.\type ("n"), .gate("br")) transistor_175 (.in(1'b0), .out(transistor_174_out), .gate(D3));
  Transistor #(.\type ("n"), .gate("br")) transistor_176 (.in(1'b0), .out(transistor_176_out), .gate(D3));
  Transistor #(.\type ("n"), .gate("br")) transistor_177 (.in(1'b0), .out(transistor_177_out), .gate(not_2_out));
  Transistor #(.\type ("n"), .gate("br")) transistor_178 (.in(1'b0), .out(transistor_177_out), .gate(D3));
  Transistor #(.\type ("n"), .gate("br")) transistor_179 (.in(1'b0), .out(transistor_179_out), .gate(D3));
  Transistor #(.\type ("n"), .gate("br")) transistor_180 (.in(1'b0), .out(transistor_180_out), .gate(D3));
  Transistor #(.\type ("n"), .gate("br")) transistor_181 (.in(1'b0), .out(transistor_180_out), .gate(not_2_out));
  Transistor #(.\type ("n"), .gate("br")) transistor_182 (.in(1'b0), .out(transistor_182_out), .gate(D3));
  Transistor #(.\type ("n"), .gate("br")) transistor_183 (.in(1'b0), .out(transistor_183_out), .gate(not_2_out));
  Transistor #(.\type ("n"), .gate("br")) transistor_184 (.in(1'b0), .out(transistor_183_out), .gate(D3));
  Transistor #(.\type ("n"), .gate("br")) transistor_185 (.in(1'b0), .out(transistor_185_out), .gate(D3));
  not not_2 (not_2_out, D4);
  Transistor #(.\type ("n"), .gate("br")) transistor_186 (.in(1'b0), .out(transistor_139_out), .gate(D4));
  Transistor #(.\type ("n"), .gate("br")) transistor_187 (.in(1'b0), .out(transistor_141_out), .gate(D4));
  Transistor #(.\type ("n"), .gate("br")) transistor_188 (.in(1'b0), .out(transistor_143_out), .gate(D4));
  Transistor #(.\type ("n"), .gate("br")) transistor_189 (.in(1'b0), .out(transistor_145_out), .gate(D4));
  Transistor #(.\type ("n"), .gate("br")) transistor_190 (.in(1'b0), .out(transistor_147_out), .gate(D4));
  Transistor #(.\type ("n"), .gate("br")) transistor_191 (.in(1'b0), .out(transistor_149_out), .gate(D4));
  Transistor #(.\type ("n"), .gate("br")) transistor_192 (.in(1'b0), .out(transistor_151_out), .gate(D4));
  Transistor #(.\type ("n"), .gate("br")) transistor_193 (.in(1'b0), .out(transistor_153_out), .gate(D4));
  Transistor #(.\type ("n"), .gate("br")) transistor_194 (.in(1'b0), .out(transistor_164_out), .gate(D4));
  Transistor #(.\type ("n"), .gate("br")) transistor_195 (.in(1'b0), .out(transistor_167_out), .gate(D4));
  Transistor #(.\type ("n"), .gate("br")) transistor_196 (.in(1'b0), .out(transistor_170_out), .gate(D4));
  Transistor #(.\type ("n"), .gate("br")) transistor_197 (.in(1'b0), .out(transistor_173_out), .gate(D4));
  Transistor #(.\type ("n"), .gate("br")) transistor_198 (.in(1'b0), .out(transistor_176_out), .gate(D4));
  Transistor #(.\type ("n"), .gate("br")) transistor_199 (.in(1'b0), .out(transistor_179_out), .gate(D4));
  Transistor #(.\type ("n"), .gate("br")) transistor_200 (.in(1'b0), .out(transistor_182_out), .gate(D4));
  Transistor #(.\type ("n"), .gate("br")) transistor_201 (.in(1'b0), .out(transistor_185_out), .gate(D4));
  Transistor #(.\type ("n"), .gate("br")) transistor_202 (.in(1'b0), .out(transistor_138_out), .gate(not_3_out));
  Transistor #(.\type ("n"), .gate("br")) transistor_203 (.in(1'b0), .out(transistor_139_out), .gate(not_3_out));
  Transistor #(.\type ("n"), .gate("br")) transistor_204 (.in(1'b0), .out(transistor_142_out), .gate(not_3_out));
  Transistor #(.\type ("n"), .gate("br")) transistor_205 (.in(1'b0), .out(transistor_143_out), .gate(not_3_out));
  Transistor #(.\type ("n"), .gate("br")) transistor_206 (.in(1'b0), .out(transistor_146_out), .gate(not_3_out));
  Transistor #(.\type ("n"), .gate("br")) transistor_207 (.in(1'b0), .out(transistor_147_out), .gate(not_3_out));
  Transistor #(.\type ("n"), .gate("br")) transistor_208 (.in(1'b0), .out(transistor_150_out), .gate(not_3_out));
  Transistor #(.\type ("n"), .gate("br")) transistor_209 (.in(1'b0), .out(transistor_151_out), .gate(not_3_out));
  Transistor #(.\type ("n"), .gate("br")) transistor_210 (.in(1'b0), .out(transistor_162_out), .gate(not_3_out));
  Transistor #(.\type ("n"), .gate("br")) transistor_211 (.in(1'b0), .out(transistor_164_out), .gate(not_3_out));
  Transistor #(.\type ("n"), .gate("br")) transistor_212 (.in(1'b0), .out(transistor_168_out), .gate(not_3_out));
  Transistor #(.\type ("n"), .gate("br")) transistor_213 (.in(1'b0), .out(transistor_170_out), .gate(not_3_out));
  Transistor #(.\type ("n"), .gate("br")) transistor_214 (.in(1'b0), .out(transistor_174_out), .gate(not_3_out));
  Transistor #(.\type ("n"), .gate("br")) transistor_215 (.in(1'b0), .out(transistor_176_out), .gate(not_3_out));
  Transistor #(.\type ("n"), .gate("br")) transistor_216 (.in(1'b0), .out(transistor_180_out), .gate(not_3_out));
  Transistor #(.\type ("n"), .gate("br")) transistor_217 (.in(1'b0), .out(transistor_182_out), .gate(not_3_out));
  not not_3 (not_3_out, D5);
  Transistor #(.\type ("n"), .gate("br")) transistor_218 (.in(1'b0), .out(transistor_140_out), .gate(D5));
  Transistor #(.\type ("n"), .gate("br")) transistor_219 (.in(1'b0), .out(transistor_141_out), .gate(D5));
  Transistor #(.\type ("n"), .gate("br")) transistor_220 (.in(1'b0), .out(transistor_144_out), .gate(D5));
  Transistor #(.\type ("n"), .gate("br")) transistor_221 (.in(1'b0), .out(transistor_145_out), .gate(D5));
  Transistor #(.\type ("n"), .gate("br")) transistor_222 (.in(1'b0), .out(transistor_148_out), .gate(D5));
  Transistor #(.\type ("n"), .gate("br")) transistor_223 (.in(1'b0), .out(transistor_149_out), .gate(D5));
  Transistor #(.\type ("n"), .gate("br")) transistor_224 (.in(1'b0), .out(transistor_152_out), .gate(D5));
  Transistor #(.\type ("n"), .gate("br")) transistor_225 (.in(1'b0), .out(transistor_153_out), .gate(D5));
  Transistor #(.\type ("n"), .gate("br")) transistor_226 (.in(1'b0), .out(transistor_165_out), .gate(D5));
  Transistor #(.\type ("n"), .gate("br")) transistor_227 (.in(1'b0), .out(transistor_167_out), .gate(D5));
  Transistor #(.\type ("n"), .gate("br")) transistor_228 (.in(1'b0), .out(transistor_171_out), .gate(D5));
  Transistor #(.\type ("n"), .gate("br")) transistor_229 (.in(1'b0), .out(transistor_173_out), .gate(D5));
  Transistor #(.\type ("n"), .gate("br")) transistor_230 (.in(1'b0), .out(transistor_177_out), .gate(D5));
  Transistor #(.\type ("n"), .gate("br")) transistor_231 (.in(1'b0), .out(transistor_179_out), .gate(D5));
  Transistor #(.\type ("n"), .gate("br")) transistor_232 (.in(1'b0), .out(transistor_183_out), .gate(D5));
  Transistor #(.\type ("n"), .gate("br")) transistor_233 (.in(1'b0), .out(transistor_185_out), .gate(D5));
  Transistor #(.\type ("n"), .gate("br")) transistor_234 (.in(1'b0), .out(transistor_138_out), .gate(not_4_out));
  Transistor #(.\type ("n"), .gate("br")) transistor_235 (.in(1'b0), .out(transistor_139_out), .gate(not_4_out));
  Transistor #(.\type ("n"), .gate("br")) transistor_236 (.in(1'b0), .out(transistor_140_out), .gate(not_4_out));
  Transistor #(.\type ("n"), .gate("br")) transistor_237 (.in(1'b0), .out(transistor_141_out), .gate(not_4_out));
  Transistor #(.\type ("n"), .gate("br")) transistor_238 (.in(1'b0), .out(transistor_146_out), .gate(not_4_out));
  Transistor #(.\type ("n"), .gate("br")) transistor_239 (.in(1'b0), .out(transistor_147_out), .gate(not_4_out));
  Transistor #(.\type ("n"), .gate("br")) transistor_240 (.in(1'b0), .out(transistor_148_out), .gate(not_4_out));
  Transistor #(.\type ("n"), .gate("br")) transistor_241 (.in(1'b0), .out(transistor_149_out), .gate(not_4_out));
  Transistor #(.\type ("n"), .gate("br")) transistor_242 (.in(1'b0), .out(transistor_162_out), .gate(not_4_out));
  Transistor #(.\type ("n"), .gate("br")) transistor_243 (.in(1'b0), .out(transistor_164_out), .gate(not_4_out));
  Transistor #(.\type ("n"), .gate("br")) transistor_244 (.in(1'b0), .out(transistor_165_out), .gate(not_4_out));
  Transistor #(.\type ("n"), .gate("br")) transistor_245 (.in(1'b0), .out(transistor_167_out), .gate(not_4_out));
  Transistor #(.\type ("n"), .gate("br")) transistor_246 (.in(1'b0), .out(transistor_174_out), .gate(not_4_out));
  Transistor #(.\type ("n"), .gate("br")) transistor_247 (.in(1'b0), .out(transistor_176_out), .gate(not_4_out));
  Transistor #(.\type ("n"), .gate("br")) transistor_248 (.in(1'b0), .out(transistor_177_out), .gate(not_4_out));
  Transistor #(.\type ("n"), .gate("br")) transistor_249 (.in(1'b0), .out(transistor_179_out), .gate(not_4_out));
  not not_4 (not_4_out, D6);
  Transistor #(.\type ("n"), .gate("br")) transistor_250 (.in(1'b0), .out(transistor_142_out), .gate(D6));
  Transistor #(.\type ("n"), .gate("br")) transistor_251 (.in(1'b0), .out(transistor_143_out), .gate(D6));
  Transistor #(.\type ("n"), .gate("br")) transistor_252 (.in(1'b0), .out(transistor_144_out), .gate(D6));
  Transistor #(.\type ("n"), .gate("br")) transistor_253 (.in(1'b0), .out(transistor_145_out), .gate(D6));
  Transistor #(.\type ("n"), .gate("br")) transistor_254 (.in(1'b0), .out(transistor_150_out), .gate(D6));
  Transistor #(.\type ("n"), .gate("br")) transistor_255 (.in(1'b0), .out(transistor_151_out), .gate(D6));
  Transistor #(.\type ("n"), .gate("br")) transistor_256 (.in(1'b0), .out(transistor_152_out), .gate(D6));
  Transistor #(.\type ("n"), .gate("br")) transistor_257 (.in(1'b0), .out(transistor_153_out), .gate(D6));
  Transistor #(.\type ("n"), .gate("br")) transistor_258 (.in(1'b0), .out(transistor_168_out), .gate(D6));
  Transistor #(.\type ("n"), .gate("br")) transistor_259 (.in(1'b0), .out(transistor_170_out), .gate(D6));
  Transistor #(.\type ("n"), .gate("br")) transistor_260 (.in(1'b0), .out(transistor_171_out), .gate(D6));
  Transistor #(.\type ("n"), .gate("br")) transistor_261 (.in(1'b0), .out(transistor_173_out), .gate(D6));
  Transistor #(.\type ("n"), .gate("br")) transistor_262 (.in(1'b0), .out(transistor_180_out), .gate(D6));
  Transistor #(.\type ("n"), .gate("br")) transistor_263 (.in(1'b0), .out(transistor_182_out), .gate(D6));
  Transistor #(.\type ("n"), .gate("br")) transistor_264 (.in(1'b0), .out(transistor_183_out), .gate(D6));
  Transistor #(.\type ("n"), .gate("br")) transistor_265 (.in(1'b0), .out(transistor_185_out), .gate(D6));
  not not_5 (not_5_out, D7);
  Transistor #(.\type ("n"), .gate("br")) transistor_266 (.in(1'b0), .out(transistor_138_out), .gate(not_5_out));
  Transistor #(.\type ("n"), .gate("br")) transistor_267 (.in(1'b0), .out(transistor_139_out), .gate(not_5_out));
  Transistor #(.\type ("n"), .gate("br")) transistor_268 (.in(1'b0), .out(transistor_140_out), .gate(not_5_out));
  Transistor #(.\type ("n"), .gate("br")) transistor_269 (.in(1'b0), .out(transistor_141_out), .gate(not_5_out));
  Transistor #(.\type ("n"), .gate("br")) transistor_270 (.in(1'b0), .out(transistor_142_out), .gate(not_5_out));
  Transistor #(.\type ("n"), .gate("br")) transistor_271 (.in(1'b0), .out(transistor_143_out), .gate(not_5_out));
  Transistor #(.\type ("n"), .gate("br")) transistor_272 (.in(1'b0), .out(transistor_144_out), .gate(not_5_out));
  Transistor #(.\type ("n"), .gate("br")) transistor_273 (.in(1'b0), .out(transistor_145_out), .gate(not_5_out));
  Transistor #(.\type ("n"), .gate("br")) transistor_274 (.in(1'b0), .out(transistor_162_out), .gate(not_5_out));
  Transistor #(.\type ("n"), .gate("br")) transistor_275 (.in(1'b0), .out(transistor_164_out), .gate(not_5_out));
  Transistor #(.\type ("n"), .gate("br")) transistor_276 (.in(1'b0), .out(transistor_165_out), .gate(not_5_out));
  Transistor #(.\type ("n"), .gate("br")) transistor_277 (.in(1'b0), .out(transistor_167_out), .gate(not_5_out));
  Transistor #(.\type ("n"), .gate("br")) transistor_278 (.in(1'b0), .out(transistor_168_out), .gate(not_5_out));
  Transistor #(.\type ("n"), .gate("br")) transistor_279 (.in(1'b0), .out(transistor_170_out), .gate(not_5_out));
  Transistor #(.\type ("n"), .gate("br")) transistor_280 (.in(1'b0), .out(transistor_171_out), .gate(not_5_out));
  Transistor #(.\type ("n"), .gate("br")) transistor_281 (.in(1'b0), .out(transistor_173_out), .gate(not_5_out));
  Pull_Resistor #(.pull(1)) pull_resistor_9 (.node(transistor_138_out));
  Pull_Resistor #(.pull(1)) pull_resistor_10 (.node(transistor_139_out));
  Pull_Resistor #(.pull(1)) pull_resistor_11 (.node(transistor_140_out));
  Pull_Resistor #(.pull(1)) pull_resistor_12 (.node(transistor_141_out));
  Pull_Resistor #(.pull(1)) pull_resistor_13 (.node(transistor_142_out));
  Pull_Resistor #(.pull(1)) pull_resistor_14 (.node(transistor_143_out));
  Pull_Resistor #(.pull(1)) pull_resistor_15 (.node(transistor_144_out));
  Pull_Resistor #(.pull(1)) pull_resistor_16 (.node(transistor_145_out));
  Pull_Resistor #(.pull(1)) pull_resistor_17 (.node(transistor_146_out));
  Transistor #(.\type ("n"), .gate("br")) transistor_282 (.in(1'b0), .out(transistor_146_out), .gate(D7));
  Transistor #(.\type ("n"), .gate("br")) transistor_283 (.in(1'b0), .out(transistor_147_out), .gate(D7));
  Pull_Resistor #(.pull(1)) pull_resistor_18 (.node(transistor_147_out));
  Transistor #(.\type ("n"), .gate("br")) transistor_284 (.in(1'b0), .out(transistor_148_out), .gate(D7));
  Pull_Resistor #(.pull(1)) pull_resistor_19 (.node(transistor_148_out));
  Pull_Resistor #(.pull(1)) pull_resistor_20 (.node(transistor_149_out));
  Transistor #(.\type ("n"), .gate("br")) transistor_285 (.in(1'b0), .out(transistor_149_out), .gate(D7));
  Pull_Resistor #(.pull(1)) pull_resistor_21 (.node(transistor_150_out));
  Transistor #(.\type ("n"), .gate("br")) transistor_286 (.in(1'b0), .out(transistor_150_out), .gate(D7));
  Pull_Resistor #(.pull(1)) pull_resistor_22 (.node(transistor_151_out));
  Transistor #(.\type ("n"), .gate("br")) transistor_287 (.in(1'b0), .out(transistor_151_out), .gate(D7));
  Transistor #(.\type ("n"), .gate("br")) transistor_288 (.in(1'b0), .out(transistor_152_out), .gate(D7));
  Pull_Resistor #(.pull(1)) pull_resistor_23 (.node(transistor_152_out));
  Pull_Resistor #(.pull(1)) pull_resistor_24 (.node(transistor_153_out));
  Transistor #(.\type ("n"), .gate("br")) transistor_289 (.in(1'b0), .out(transistor_153_out), .gate(D7));
  Pull_Resistor #(.pull(1)) pull_resistor_25 (.node(transistor_162_out));
  Pull_Resistor #(.pull(1)) pull_resistor_26 (.node(transistor_164_out));
  Pull_Resistor #(.pull(1)) pull_resistor_27 (.node(transistor_165_out));
  Pull_Resistor #(.pull(1)) pull_resistor_28 (.node(transistor_167_out));
  Pull_Resistor #(.pull(1)) pull_resistor_29 (.node(transistor_168_out));
  Pull_Resistor #(.pull(1)) pull_resistor_30 (.node(transistor_170_out));
  Pull_Resistor #(.pull(1)) pull_resistor_31 (.node(transistor_171_out));
  Pull_Resistor #(.pull(1)) pull_resistor_32 (.node(transistor_173_out));
  Transistor #(.\type ("n"), .gate("br")) transistor_290 (.in(1'b0), .out(transistor_174_out), .gate(D7));
  Pull_Resistor #(.pull(1)) pull_resistor_33 (.node(transistor_174_out));
  Pull_Resistor #(.pull(1)) pull_resistor_34 (.node(transistor_176_out));
  Transistor #(.\type ("n"), .gate("br")) transistor_291 (.in(1'b0), .out(transistor_176_out), .gate(D7));
  Pull_Resistor #(.pull(1)) pull_resistor_35 (.node(transistor_177_out));
  Transistor #(.\type ("n"), .gate("br")) transistor_292 (.in(1'b0), .out(transistor_177_out), .gate(D7));
  Transistor #(.\type ("n"), .gate("br")) transistor_293 (.in(1'b0), .out(transistor_179_out), .gate(D7));
  Pull_Resistor #(.pull(1)) pull_resistor_36 (.node(transistor_179_out));
  Transistor #(.\type ("n"), .gate("br")) transistor_294 (.in(1'b0), .out(transistor_180_out), .gate(D7));
  Pull_Resistor #(.pull(1)) pull_resistor_37 (.node(transistor_180_out));
  Pull_Resistor #(.pull(1)) pull_resistor_38 (.node(transistor_182_out));
  Transistor #(.\type ("n"), .gate("br")) transistor_295 (.in(1'b0), .out(transistor_182_out), .gate(D7));
  Transistor #(.\type ("n"), .gate("br")) transistor_296 (.in(1'b0), .out(transistor_183_out), .gate(D7));
  Pull_Resistor #(.pull(1)) pull_resistor_39 (.node(transistor_183_out));
  Transistor #(.\type ("n"), .gate("br")) transistor_297 (.in(1'b0), .out(transistor_185_out), .gate(D7));
  Pull_Resistor #(.pull(1)) pull_resistor_40 (.node(transistor_185_out));

  // Notes on the sheet:
  //   /D3
  //   D3
  //   /D4
  //   D4
  //   /D5
  //   D5
  //   /D6
  //   D6
  //   /D7
  //   D7
  //   8
  //   7
  //   6
  //   5
  //   4
  //   3
  //   2
  //   1
  //   8
  //   7
  //   6
  //   5
  //   4
  //   3
  //   2
  //   1
  //   8
  //   7
  //   6
  //   5
  //   4
  //   3
  //   2
  //   1
  //   8
  //   7
  //   6
  //   5
  //   4
  //   3
  //   2
  //   1
endmodule

module DLATCH (
  input  EN,
  input  IN,
  output Q,
  output nQ
);

  D_Flip_Flop #(.trigger("high")) d_ff_1 (.clk(EN), .D(IN), .Q(Q), .Qn(nQ));  // open: preset, en, reset
endmodule

module DLATCHres (
  input  EN,
  input  IN,
  input  Res,
  output Q,
  output nQ
);

  D_Flip_Flop #(.trigger("high")) d_ff_1 (.clk(EN), .D(IN), .Q(Q), .Qn(nQ), .reset(Res));  // open: preset, en
endmodule

module CounterCell (
  input  nACLK,
  input  ACLK,
  input  LCX,
  input  W4003,
  input  STEP,
  input  RES,
  input  Carry_In,
  output Carry_Out
);

  wire controlled_buffer_1_out, dlatch_1_nq, dlatchres_1_nq, dlatchres_1_q, multiplexer_1_out, not_1_out;

  assign controlled_buffer_1_out = W4003 ? LCX : 1'bz;  // Controlled_Buffer controlled_buffer_1
  assign controlled_buffer_1_out = STEP ? dlatch_1_nq : 1'bz;  // Controlled_Buffer controlled_buffer_2
  DLATCHres dlatchres_1 (.EN(ACLK), .IN(controlled_buffer_1_out), .Res(RES), .Q(dlatchres_1_q), .nQ(dlatchres_1_nq));
  not not_1 (not_1_out, Carry_In);
  DLATCH dlatch_1 (.EN(nACLK), .IN(multiplexer_1_out), .nQ(dlatch_1_nq));  // open: Q
  Multiplexer multiplexer_1 (
    .in0(dlatchres_1_nq), .in1(dlatchres_1_q), .out(multiplexer_1_out), .sel(Carry_In));  // open: en
  nor nor_1 (Carry_Out, dlatchres_1_q, not_1_out);
endmodule

module ControlUnit (
  input  ACLK,
  input  nACLK,
  input  W4003,
  input  Carry_In,
  input  W4015,
  input  D0,
  input  Res,
  input  nLFO2,
  input  nR4015,
  output NOSQA,
  output D0_2,
  output STEP
);

  wire and_1_out, and_2_out, and_3_out, d_ff_1_q, d_ff_2_qn, d_ff_3_q, d_ff_4_q, nor_2_out, nor_3_out,
       not_1_out, not_2_out;

  D_Flip_Flop d_ff_1 (.clk(nACLK), .D(Carry_In), .Q(d_ff_1_q));  // open: Qn, preset, en, reset
  and and_1 (and_1_out, ACLK, W4015);
  D_Flip_Flop d_ff_2 (.clk(and_1_out), .D(D0), .Qn(d_ff_2_qn), .reset(Res));  // open: Q, preset, en
  not not_1 (not_1_out, ACLK);
  D_Flip_Flop d_ff_3 (.clk(nACLK), .D(d_ff_2_qn), .Q(d_ff_3_q));  // open: Qn, preset, en, reset
  nor nor_1 (STEP, nLFO2, d_ff_4_q);
  and and_2 (and_2_out, d_ff_1_q, STEP);
  and and_3 (and_3_out, not_1_out, d_ff_3_q);
  not not_2 (not_2_out, nR4015);
  not not_3 (NOSQA, nor_2_out);
  nor nor_2 (nor_2_out, Res, and_2_out, and_3_out, nor_3_out);
  nor nor_3 (nor_3_out, nor_2_out, W4003);
  assign D0_2 = not_2_out ? ~nor_3_out : 1'bz;  // Controlled_Inverter controlled_inverter_1
  D_Flip_Flop d_ff_4 (.clk(nACLK), .D(nor_3_out), .Q(d_ff_4_q));  // open: Qn, preset, en, reset

  // Notes on the sheet:
  //   /ACLK1
endmodule

module Masterclock (
  input  PHI0,
  input  RES,
  output PHI1,
  output PHI2,
  output ACLK,
  output nACLK
);

  wire d_ff_1_qn, d_ff_2_qn, nor_1_out, nor_2_out, not_2_out;

  not not_1 (PHI1, PHI0);
  not not_2 (not_2_out, PHI1);
  D_Flip_Flop d_ff_1 (.clk(PHI1), .D(nor_1_out), .Qn(d_ff_1_qn));  // open: Q, preset, en, reset
  D_Flip_Flop d_ff_2 (.clk(PHI0), .D(d_ff_1_qn), .Qn(d_ff_2_qn));  // open: Q, preset, en, reset
  nor nor_1 (nor_1_out, d_ff_2_qn, RES);
  nor nor_2 (nor_2_out, nor_1_out, not_2_out);
  nor nor_3 (nACLK, not_2_out, PHI0, d_ff_2_qn);
  not not_3 (ACLK, nor_2_out);

  assign PHI2 = PHI0;

  // Notes on the sheet:
  //   INV1
  //   DL1
  //   DL2
  //   NOR1
  //   NOR2
  //   NOR3
endmodule

module Counter (
  input  nACLK,
  input  STEP,
  input  W4003,
  input  D3,
  input  D4,
  input  D5,
  input  D6,
  input  D7,
  input  HALT,
  input  RES,
  output Carry_Out
);

  wire and_1_out, and_2_out, and_3_out, and_4_out, and_5_out, and_6_out, and_7_out, and_8_out, and_9_out,
       and_10_out, and_11_out, and_12_out, and_13_out, and_14_out, and_15_out, and_16_out, d_ff_1_q,
       d_ff_1_qn, d_ff_2_q, d_ff_2_qn, d_ff_3_q, d_ff_3_qn, d_ff_4_q, d_ff_4_qn, d_ff_5_q, d_ff_5_qn,
       d_ff_6_q, d_ff_6_qn, d_ff_7_q, d_ff_7_qn, d_ff_8_q, d_ff_8_qn, d_ff_9_qn, d_ff_10_qn, d_ff_11_qn,
       d_ff_12_qn, d_ff_13_qn, d_ff_14_qn, d_ff_15_qn, d_ff_16_qn, decoder_1_lc0, decoder_1_lc1,
       decoder_1_lc2, decoder_1_lc3, decoder_1_lc4, decoder_1_lc5, decoder_1_lc6, decoder_1_lc7,
       multiplexer_1_out, multiplexer_2_out, multiplexer_3_out, multiplexer_4_out, multiplexer_5_out,
       multiplexer_6_out, multiplexer_7_out, multiplexer_8_out, nor_2_out, nor_3_out, nor_4_out, nor_5_out,
       nor_6_out, nor_7_out, nor_8_out, not_1_out, not_2_out, not_3_out, not_4_out, not_5_out, not_6_out,
       not_7_out, not_8_out, not_9_out, not_10_out, not_11_out, not_12_out, not_13_out, not_14_out,
       not_15_out, not_16_out, or_1_out, or_2_out, or_3_out, or_4_out, or_5_out, or_6_out, or_7_out, or_8_out;

  Decoder decoder_1 (
    .D3(D3), .D4(D4), .D5(D5), .D6(D6), .D7(D7), .LC0(decoder_1_lc0), .LC1(decoder_1_lc1),
    .LC2(decoder_1_lc2), .LC3(decoder_1_lc3), .LC4(decoder_1_lc4), .LC5(decoder_1_lc5), .LC6(decoder_1_lc6),
    .LC7(decoder_1_lc7));
  not not_1 (not_1_out, decoder_1_lc7);
  not not_2 (not_2_out, decoder_1_lc6);
  not not_3 (not_3_out, decoder_1_lc5);
  not not_4 (not_4_out, decoder_1_lc4);
  not not_5 (not_5_out, decoder_1_lc3);
  not not_6 (not_6_out, decoder_1_lc2);
  not not_7 (not_7_out, decoder_1_lc1);
  not not_8 (not_8_out, decoder_1_lc0);
  and and_1 (and_1_out, W4003, decoder_1_lc7);
  and and_2 (and_2_out, W4003, not_1_out);
  and and_3 (and_3_out, W4003, decoder_1_lc6);
  and and_4 (and_4_out, W4003, not_2_out);
  and and_5 (and_5_out, W4003, decoder_1_lc5);
  and and_6 (and_6_out, W4003, not_3_out);
  and and_7 (and_7_out, W4003, decoder_1_lc4);
  and and_8 (and_8_out, W4003, not_4_out);
  and and_9 (and_9_out, W4003, decoder_1_lc3);
  and and_10 (and_10_out, W4003, not_5_out);
  and and_11 (and_11_out, W4003, decoder_1_lc2);
  and and_12 (and_12_out, W4003, not_6_out);
  and and_13 (and_13_out, W4003, decoder_1_lc1);
  and and_14 (and_14_out, W4003, not_7_out);
  and and_15 (and_15_out, W4003, decoder_1_lc0);
  and and_16 (and_16_out, W4003, not_8_out);
  D_Flip_Flop d_ff_1 (
    .clk(STEP), .D(d_ff_9_qn), .Q(d_ff_1_q), .Qn(d_ff_1_qn), .preset(and_1_out), .reset(or_1_out));  // open: en
  or or_1 (or_1_out, and_2_out, RES);
  D_Flip_Flop d_ff_2 (
    .clk(STEP), .D(d_ff_10_qn), .Q(d_ff_2_q), .Qn(d_ff_2_qn), .preset(and_3_out), .reset(or_2_out));  // open: en
  or or_2 (or_2_out, and_4_out, RES);
  D_Flip_Flop d_ff_3 (
    .clk(STEP), .D(d_ff_11_qn), .Q(d_ff_3_q), .Qn(d_ff_3_qn), .preset(and_5_out), .reset(or_3_out));  // open: en
  or or_3 (or_3_out, and_6_out, RES);
  D_Flip_Flop d_ff_4 (
    .clk(STEP), .D(d_ff_12_qn), .Q(d_ff_4_q), .Qn(d_ff_4_qn), .preset(and_7_out), .reset(or_4_out));  // open: en
  or or_4 (or_4_out, and_8_out, RES);
  D_Flip_Flop d_ff_5 (
    .clk(STEP), .D(d_ff_13_qn), .Q(d_ff_5_q), .Qn(d_ff_5_qn), .preset(and_9_out), .reset(or_5_out));  // open: en
  or or_5 (or_5_out, and_10_out, RES);
  D_Flip_Flop d_ff_6 (
    .clk(STEP), .D(d_ff_14_qn), .Q(d_ff_6_q), .Qn(d_ff_6_qn), .preset(and_11_out), .reset(or_6_out));  // open: en
  or or_6 (or_6_out, and_12_out, RES);
  D_Flip_Flop d_ff_7 (
    .clk(STEP), .D(d_ff_15_qn), .Q(d_ff_7_q), .Qn(d_ff_7_qn), .preset(and_13_out), .reset(or_7_out));  // open: en
  or or_7 (or_7_out, and_14_out, RES);
  D_Flip_Flop d_ff_8 (
    .clk(STEP), .D(d_ff_16_qn), .Q(d_ff_8_q), .Qn(d_ff_8_qn), .preset(and_15_out), .reset(or_8_out));  // open: en
  or or_8 (or_8_out, and_16_out, RES);
  Multiplexer multiplexer_1 (.in0(d_ff_1_qn), .in1(d_ff_1_q), .out(multiplexer_1_out), .sel(nor_2_out));  // open: en
  not not_9 (not_9_out, nor_2_out);
  Multiplexer multiplexer_2 (.in0(d_ff_2_qn), .in1(d_ff_2_q), .out(multiplexer_2_out), .sel(nor_3_out));  // open: en
  not not_10 (not_10_out, nor_3_out);
  Multiplexer multiplexer_3 (.in0(d_ff_3_qn), .in1(d_ff_3_q), .out(multiplexer_3_out), .sel(nor_4_out));  // open: en
  not not_11 (not_11_out, nor_4_out);
  Multiplexer multiplexer_4 (.in0(d_ff_4_qn), .in1(d_ff_4_q), .out(multiplexer_4_out), .sel(nor_5_out));  // open: en
  not not_12 (not_12_out, nor_5_out);
  Multiplexer multiplexer_5 (.in0(d_ff_5_qn), .in1(d_ff_5_q), .out(multiplexer_5_out), .sel(nor_6_out));  // open: en
  not not_13 (not_13_out, nor_6_out);
  Multiplexer multiplexer_6 (.in0(d_ff_6_qn), .in1(d_ff_6_q), .out(multiplexer_6_out), .sel(nor_7_out));  // open: en
  not not_14 (not_14_out, nor_7_out);
  Multiplexer multiplexer_7 (.in0(d_ff_7_qn), .in1(d_ff_7_q), .out(multiplexer_7_out), .sel(nor_8_out));  // open: en
  not not_15 (not_15_out, nor_8_out);
  Multiplexer multiplexer_8 (.in0(d_ff_8_qn), .in1(d_ff_8_q), .out(multiplexer_8_out), .sel(HALT));  // open: en
  not not_16 (not_16_out, HALT);
  D_Flip_Flop d_ff_9 (.clk(nACLK), .D(multiplexer_1_out), .Qn(d_ff_9_qn));  // open: Q, preset, en, reset
  D_Flip_Flop d_ff_10 (.clk(nACLK), .D(multiplexer_2_out), .Qn(d_ff_10_qn));  // open: Q, preset, en, reset
  D_Flip_Flop d_ff_11 (.clk(nACLK), .D(multiplexer_3_out), .Qn(d_ff_11_qn));  // open: Q, preset, en, reset
  D_Flip_Flop d_ff_12 (.clk(nACLK), .D(multiplexer_4_out), .Qn(d_ff_12_qn));  // open: Q, preset, en, reset
  D_Flip_Flop d_ff_13 (.clk(nACLK), .D(multiplexer_5_out), .Qn(d_ff_13_qn));  // open: Q, preset, en, reset
  D_Flip_Flop d_ff_14 (.clk(nACLK), .D(multiplexer_6_out), .Qn(d_ff_14_qn));  // open: Q, preset, en, reset
  D_Flip_Flop d_ff_15 (.clk(nACLK), .D(multiplexer_7_out), .Qn(d_ff_15_qn));  // open: Q, preset, en, reset
  D_Flip_Flop d_ff_16 (.clk(nACLK), .D(multiplexer_8_out), .Qn(d_ff_16_qn));  // open: Q, preset, en, reset
  nor nor_1 (Carry_Out, d_ff_1_q, not_9_out);
  nor nor_2 (nor_2_out, d_ff_2_q, not_10_out);
  nor nor_3 (nor_3_out, d_ff_3_q, not_11_out);
  nor nor_4 (nor_4_out, d_ff_4_q, not_12_out);
  nor nor_5 (nor_5_out, d_ff_5_q, not_13_out);
  nor nor_6 (nor_6_out, d_ff_6_q, not_14_out);
  nor nor_7 (nor_7_out, d_ff_7_q, not_15_out);
  nor nor_8 (nor_8_out, d_ff_8_q, not_16_out);
endmodule
