// Logisim project Lfov2.circ as structural Verilog: 3 circuits, main circuit main
module main (
  input  W4017,
  input  D7,
  input  D6,
  input  Res,
  input  nR4015,
  input  DMCINT,
  output ACLK,
  output nACLK,
  output nLFO1,
  output nLFO2,
  output out_11,
  output INT,
  output D6_State
);

  wire and_1_out, and_2_out, and_3_out, and_4_out, and_5_out, CLK_out, d_ff_1_qn, d_ff_2_q, d_ff_3_q,
       d_ff_4_qn, d_ff_5_qn, d_positive_1_nout, d_positive_1_out, d_positive_2_nout, d_positive_2_out,
       d_positive_3_nout, d_positive_3_out, d_positive_4_nout, d_positive_4_out, d_positive_5_nout,
       d_positive_5_out, d_positive_6_nout, d_positive_6_out, d_positive_7_nout, d_positive_7_out,
       d_positive_8_nout, d_positive_8_out, d_positive_9_nout, d_positive_9_out, d_positive_10_nout,
       d_positive_10_out, d_positive_11_nout, d_positive_11_out, d_positive_12_nout, d_positive_12_out,
       d_positive_13_nout, d_positive_13_out, d_positive_14_nout, d_positive_14_out, d_positive_15_nout,
       d_positive_15_out, dlatch_1_nout, dlatch_2_out, dlatch_3_out, dlatch_4_nout, dlatch_5_nout,
       dlatch_6_nout, multiplexer_1_out, multiplexer_2_out, multiplexer_3_out, multiplexer_4_out,
       multiplexer_5_out, multiplexer_6_out, multiplexer_7_out, multiplexer_8_out, multiplexer_9_out,
       multiplexer_10_out, multiplexer_11_out, multiplexer_12_out, multiplexer_13_out, multiplexer_14_out,
       multiplexer_15_out, Nor1_out, Nor2_out, Nor3_out, Nor4_out, Nor5_out, nor_1_out, nor_2_out, nor_3_out,
       nor_4_out, nor_5_out, nor_6_out, nor_7_out, nor_8_out, nor_9_out, nor_10_out, nor_11_out, not_1_out,
       not_2_out, not_3_out, not_4_out, or_1_out, pull_resistor_1_node, undriven;

  and and_1 (and_1_out, ACLK, W4017);
  and and_2 (and_2_out, ACLK, W4017);
  D_Flip_Flop #(.trigger("high")) d_ff_1 (.clk(and_1_out), .D(D7), .Qn(d_ff_1_qn));  // open: Q, preset, en, reset
  D_Flip_Flop #(.trigger("high")) d_ff_2 (.clk(and_2_out), .D(D6), .Q(d_ff_2_q));  // open: Qn, preset, en, reset
  DLATCH dlatch_1 (.EN(nACLK), .in(d_ff_1_qn), .nout(dlatch_1_nout));  // open: out
  nor nor_1 (nor_1_out, nor_3_out, nor_2_out);
  nor nor_2 (nor_2_out, nor_1_out, W4017, Res);
  D_Flip_Flop #(.trigger("high")) d_ff_3 (.clk(ACLK), .D(nor_2_out), .Q(d_ff_3_q));  // open: Qn, preset, en, reset
  nor nor_3 (nor_3_out, nACLK, d_ff_3_q);
  D_Flip_Flop #(.trigger("high")) d_ff_4 (.clk(nACLK), .D(nor_2_out), .Qn(d_ff_4_qn));  // open: Q, preset, en, reset
  Clock CLK (.out(CLK_out));
  or or_1 (or_1_out, Nor2_out, Nor1_out, d_ff_4_qn);
  not not_1 (not_1_out, CLK_out);
  DLATCH dlatch_2 (.EN(nACLK), .in(d_ff_1_qn), .out(dlatch_2_out));  // open: nout
  DLATCH dlatch_3 (.EN(nACLK), .in(nor_2_out), .out(dlatch_3_out));  // open: nout
  DLATCH dlatch_4 (.EN(CLK_out), .in(1'b0), .nout(dlatch_4_nout));  // open: out
  DLATCH dlatch_5 (.EN(not_1_out), .in(dlatch_4_nout), .nout(dlatch_5_nout));  // open: out
  Multiplexer multiplexer_1 (.in0(nor_9_out), .in1(1'b1), .out(multiplexer_1_out), .sel(or_1_out));  // open: en
  Multiplexer multiplexer_2 (.in0(d_positive_1_out), .in1(1'b1), .out(multiplexer_2_out), .sel(or_1_out));  // open: en
  Multiplexer multiplexer_3 (.in0(d_positive_2_out), .in1(1'b1), .out(multiplexer_3_out), .sel(or_1_out));  // open: en
  Multiplexer multiplexer_4 (.in0(d_positive_3_out), .in1(1'b1), .out(multiplexer_4_out), .sel(or_1_out));  // open: en
  Multiplexer multiplexer_5 (.in0(d_positive_4_out), .in1(1'b1), .out(multiplexer_5_out), .sel(or_1_out));  // open: en
  Multiplexer multiplexer_6 (.in0(d_positive_5_out), .in1(1'b1), .out(multiplexer_6_out), .sel(or_1_out));  // open: en
  Multiplexer multiplexer_7 (.in0(d_positive_6_out), .in1(1'b1), .out(multiplexer_7_out), .sel(or_1_out));  // open: en
  Multiplexer multiplexer_8 (.in0(d_positive_7_out), .in1(1'b1), .out(multiplexer_8_out), .sel(or_1_out));  // open: en
  Multiplexer multiplexer_9 (.in0(d_positive_8_out), .in1(1'b1), .out(multiplexer_9_out), .sel(or_1_out));  // open: en
  Multiplexer multiplexer_10 (
    .in0(d_positive_9_out), .in1(1'b1), .out(multiplexer_10_out), .sel(or_1_out));  // open: en
  Multiplexer multiplexer_11 (
    .in0(d_positive_10_out), .in1(1'b1), .out(multiplexer_11_out), .sel(or_1_out));  // open: en
  Multiplexer multiplexer_12 (
    .in0(d_positive_11_out), .in1(1'b1), .out(multiplexer_12_out), .sel(or_1_out));  // open: en
  Multiplexer multiplexer_13 (
    .in0(d_positive_12_out), .in1(1'b1), .out(multiplexer_13_out), .sel(or_1_out));  // open: en
  Multiplexer multiplexer_14 (
    .in0(d_positive_13_out), .in1(1'b1), .out(multiplexer_14_out), .sel(or_1_out));  // open: en
  Multiplexer multiplexer_15 (
    .in0(d_positive_14_out), .in1(1'b1), .out(multiplexer_15_out), .sel(or_1_out));  // open: en
  nor nor_4 (nor_4_out, dlatch_2_out, dlatch_3_out);
  and and_3 (and_3_out, nACLK, d_ff_5_qn);
  not not_2 (not_2_out, dlatch_5_nout);
  D_positive d_positive_1 (.EN(and_3_out), .in(multiplexer_1_out), .out(d_positive_1_out), .nout(d_positive_1_nout));
  D_positive d_positive_2 (.EN(and_3_out), .in(multiplexer_2_out), .out(d_positive_2_out), .nout(d_positive_2_nout));
  D_positive d_positive_3 (.EN(and_3_out), .in(multiplexer_3_out), .out(d_positive_3_out), .nout(d_positive_3_nout));
  D_positive d_positive_4 (.EN(and_3_out), .in(multiplexer_4_out), .out(d_positive_4_out), .nout(d_positive_4_nout));
  D_positive d_positive_5 (.EN(and_3_out), .in(multiplexer_5_out), .out(d_positive_5_out), .nout(d_positive_5_nout));
  D_positive d_positive_6 (.EN(and_3_out), .in(multiplexer_6_out), .out(d_positive_6_out), .nout(d_positive_6_nout));
  D_positive d_positive_7 (.EN(and_3_out), .in(multiplexer_7_out), .out(d_positive_7_out), .nout(d_positive_7_nout));
  D_positive d_positive_8 (.EN(and_3_out), .in(multiplexer_8_out), .out(d_positive_8_out), .nout(d_positive_8_nout));
  D_positive d_positive_9 (.EN(and_3_out), .in(multiplexer_9_out), .out(d_positive_9_out), .nout(d_positive_9_nout));
  D_positive d_positive_10 (
    .EN(and_3_out), .in(multiplexer_10_out), .out(d_positive_10_out), .nout(d_positive_10_nout));
  D_positive d_positive_11 (
    .EN(and_3_out), .in(multiplexer_11_out), .out(d_positive_11_out), .nout(d_positive_11_nout));
  D_positive d_positive_12 (
    .EN(and_3_out), .in(multiplexer_12_out), .out(d_positive_12_out), .nout(d_positive_12_nout));
  D_positive d_positive_13 (
    .EN(and_3_out), .in(multiplexer_13_out), .out(d_positive_13_out), .nout(d_positive_13_nout));
  D_positive d_positive_14 (
    .EN(and_3_out), .in(multiplexer_14_out), .out(d_positive_14_out), .nout(d_positive_14_nout));
  D_positive d_positive_15 (
    .EN(and_3_out), .in(multiplexer_15_out), .out(d_positive_15_out), .nout(d_positive_15_nout));
  Multiplexer multiplexer_16 (.in0(1'b0), .in1(not_2_out), .out(nACLK), .sel(CLK_out));  // open: en
  not not_3 (not_3_out, CLK_out);
  and and_4 (and_4_out, Nor2_out, d_ff_1_qn);
  nor nor_5 (nor_5_out, CLK_out, nR4015);
  Multiplexer multiplexer_17 (.in0(not_3_out), .in1(1'b0), .out(ACLK), .sel(1'b0));  // open: en
  nor nor_6 (nor_6_out, and_4_out, nor_7_out);
  nor nor_7 (nor_7_out, nor_6_out, d_ff_2_q, Res, nor_5_out);
  DLATCH dlatch_6 (.EN(nACLK), .in(nor_6_out), .nout(dlatch_6_nout));  // open: out
  nor Nor1 (Nor1_out, d_positive_1_nout, d_positive_2_out, d_positive_3_nout, d_positive_4_out, d_positive_5_out, d_positive_6_out, d_positive_7_out, d_positive_8_nout, d_positive_9_nout, d_positive_10_out, d_positive_11_out, d_positive_12_out, d_positive_13_nout, d_positive_14_nout, d_positive_15_nout);
  nor Nor0 (out_11, d_positive_1_out, d_positive_2_out, d_positive_3_out, d_positive_4_out, d_positive_5_out, d_positive_6_out, d_positive_7_out, d_positive_8_out, d_positive_9_out, d_positive_10_out, d_positive_11_out, d_positive_12_out, d_positive_13_out, d_positive_14_out, d_positive_15_out);
  not not_4 (not_4_out, nR4015);
  nor Nor2 (Nor2_out, d_positive_8_out, d_positive_1_nout, d_positive_2_nout, d_positive_3_nout, d_positive_4_nout, d_positive_5_nout, d_positive_6_out, d_positive_7_out, d_positive_9_out, d_positive_10_nout, d_positive_11_out, d_positive_12_nout, d_positive_13_out, d_positive_14_out, d_positive_15_out, dlatch_1_nout);
  assign D6_State = not_4_out ? dlatch_6_nout : 1'bz;  // Controlled_Buffer controlled_buffer_1
  nor Nor5 (Nor5_out, d_positive_1_nout, d_positive_2_out, d_positive_3_out, d_positive_4_out, d_positive_5_out, d_positive_6_nout, d_positive_7_nout, d_positive_8_out, d_positive_9_out, d_positive_10_out, d_positive_11_out, d_positive_12_out, d_positive_13_nout, d_positive_14_out, d_positive_15_out);
  nor Nor4 (Nor4_out, d_positive_1_nout, d_positive_2_nout, d_positive_3_out, d_positive_4_out, d_positive_5_out, d_positive_6_out, d_positive_7_out, d_positive_8_out, d_positive_9_out, d_positive_10_nout, d_positive_11_nout, d_positive_12_out, d_positive_13_nout, d_positive_14_nout, d_positive_15_out);
  nor Nor3 (Nor3_out, d_positive_1_nout, d_positive_2_nout, d_positive_3_out, d_positive_4_out, d_positive_5_nout, d_positive_6_out, d_positive_7_nout, d_positive_8_nout, d_positive_9_out, d_positive_10_out, d_positive_11_nout, d_positive_12_nout, d_positive_13_out, d_positive_14_nout, d_positive_15_out);
  or or_2 (INT, nor_7_out, DMCINT);
  nor nor_8 (nor_8_out, out_11, d_positive_15_out, d_positive_14_out);
  nor nor_9 (nor_9_out, nor_8_out, and_5_out);
  and and_5 (and_5_out, d_positive_15_out, d_positive_14_out);
  nor nor_10 (nor_10_out, Nor5_out, Nor4_out, Nor3_out, Nor2_out, Nor1_out, nor_4_out);
  nor nor_11 (nor_11_out, Nor2_out, Nor4_out, Nor1_out, nor_4_out);
  Pull_Resistor #(.pull(1)) pull_resistor_1 (.node(pull_resistor_1_node));
  D_Flip_Flop d_ff_5 (
    .clk(undriven), .D(pull_resistor_1_node), .Qn(d_ff_5_qn), .reset(d_ff_4_qn));  // open: Q, preset, en
  or or_3 (nLFO1, ACLK, nor_10_out);
  or or_4 (nLFO2, ACLK, nor_11_out);
  Counter #(.width(28), .max('hfffffff), .trigger("falling")) counter_1 (
    .clk(nLFO2), .clr(d_ff_4_qn));  // open: load, D, count, Q, carry
  Counter #(.width(22), .max('h3fffff)) counter_2 (.clk(and_3_out), .clr(d_ff_4_qn));  // open: load, D, count, Q, carry

  // Notes on the sheet:
  //   PHI1
  //   PHI2
  //   0
  //   1
  //   2
  //   3
  //   4
  //   5
  //   6
  //   7
  //   8
  //   9
  //   10
  //   11
  //   12
  //   13
  //   14
  //   Nor3=11185
  //   Nor2=14914
  //   Nor1=18640
  //   Nor5=3728
  //   Nor4=7456
  //   Connect as original
endmodule

module DLATCH (
  input  EN,
  input  in,
  output out,
  output nout
);

  D_Flip_Flop #(.trigger("high")) d_ff_1 (.clk(EN), .D(in), .Q(out), .Qn(nout));  // open: preset, en, reset
endmodule

module D_positive (
  input  EN,
  input  in,
  output out,
  output nout
);

  D_Flip_Flop d_ff_1 (.clk(EN), .D(in), .Q(out), .Qn(nout));  // open: preset, en, reset
endmodule
