// Logisim project Lfov2rev.circ as structural Verilog: 4 circuits, main circuit main
module main (
  input  in_1,
  input  W4017,
  input  D7,
  input  D6,
  input  Res,
  input  nR4015,
  input  DMCINT,
  output PHI1,
  output PHI2,
  output ACLK,
  output nACLK,
  output nLFO1,
  output nLFO2,
  output out_14,
  output INT,
  output D6_State
);

  wire and_1_out, and_2_out, and_3_out, and_4_out, clock_1_out, d_ff_1_qn, d_ff_2_q, d_ff_3_qn, d_ff_4_q,
       d_ff_5_qn, d_ff_6_q, d_ff_7_q, d_ff_8_q, d_ff_9_q, d_ff_10_q, d_ff_11_q, d_ff_12_q, d_ff_13_q,
       d_ff_14_q, d_ff_15_q, d_ff_16_q, d_ff_17_q, d_ff_18_q, d_ff_19_q, d_ff_20_q, d_ff_21_q, d_ff_22_q,
       d_ff_23_q, d_ff_23_qn, d_ff_24_q, d_ff_24_qn, d_ff_25_q, d_ff_25_qn, d_ff_26_q, d_ff_26_qn, d_ff_27_q,
       d_ff_27_qn, d_ff_28_q, d_ff_28_qn, d_ff_29_q, d_ff_29_qn, d_ff_30_q, d_ff_30_qn, d_ff_31_q,
       d_ff_31_qn, d_ff_32_q, d_ff_32_qn, d_ff_33_q, d_ff_33_qn, d_ff_34_q, d_ff_34_qn, d_ff_35_q,
       d_ff_35_qn, d_ff_36_q, d_ff_36_qn, d_ff_37_q, d_ff_37_qn, d_ff_38_qn, Nor1_out, Nor2_out, Nor3_out,
       Nor4_out, Nor5_out, nor_1_out, nor_2_out, nor_3_out, nor_4_out, nor_5_out, nor_6_out, nor_7_out,
       nor_8_out, nor_9_out, nor_10_out, nor_11_out, nor_12_out, nor_13_out, nor_14_out, nor_15_out,
       nor_16_out, nor_17_out, not_1_out, not_2_out, not_4_out;
  wire [15:0] counter_1_q, counter_2_q, counter_3_q, register_3_q;

  and and_1 (and_1_out, ACLK, W4017);
  and and_2 (and_2_out, ACLK, W4017);
  D_Flip_Flop #(.trigger("high")) d_ff_1 (.clk(and_1_out), .D(D7), .Qn(d_ff_1_qn));  // open: Q, preset, en, reset
  D_Flip_Flop #(.trigger("high")) d_ff_2 (.clk(and_2_out), .D(D6), .Q(d_ff_2_q));  // open: Qn, preset, en, reset
  nor nor_1 (nor_1_out, nor_3_out, nor_2_out);
  nor nor_2 (nor_2_out, nor_1_out, W4017, Res);
  D_Flip_Flop d_ff_3 (.clk(nACLK), .D(d_ff_1_qn), .Qn(d_ff_3_qn));  // open: Q, preset, en, reset
  D_Flip_Flop d_ff_4 (.clk(nACLK), .D(nor_2_out), .Q(d_ff_4_q));  // open: Qn, preset, en, reset
  Clock clock_1 (.out(clock_1_out));
  nor nor_3 (nor_3_out, ACLK, d_ff_4_q);
  D_Flip_Flop d_ff_5 (.clk(nACLK), .D(nor_2_out), .Qn(d_ff_5_qn));  // open: Q, preset, en, reset
  not not_1 (not_1_out, nor_4_out);
  nor nor_4 (nor_4_out, Nor2_out, Nor1_out, d_ff_5_qn);
  Masterclock masterclock_1 (.PHI0(clock_1_out), .RES(Res), .PHI1(PHI1), .PHI2(PHI2), .ACLK(ACLK), .nACLK(nACLK));
  nor nor_5 (nor_5_out, ACLK, not_1_out);
  nor nor_6 (nor_6_out, ACLK, nor_4_out);
  D_Flip_Flop d_ff_6 (.clk(nACLK), .D(d_ff_1_qn), .Q(d_ff_6_q));  // open: Qn, preset, en, reset
  D_Flip_Flop d_ff_7 (.clk(nACLK), .D(nor_2_out), .Q(d_ff_7_q));  // open: Qn, preset, en, reset
  D_Flip_Flop d_ff_8 (.clk(nor_5_out), .D(nor_13_out), .Q(d_ff_8_q), .preset(nor_6_out));  // open: Qn, en, reset
  D_Flip_Flop d_ff_9 (.clk(nor_5_out), .D(d_ff_23_q), .Q(d_ff_9_q), .preset(nor_6_out));  // open: Qn, en, reset
  D_Flip_Flop d_ff_10 (.clk(nor_5_out), .D(d_ff_24_q), .Q(d_ff_10_q), .preset(nor_6_out));  // open: Qn, en, reset
  D_Flip_Flop d_ff_11 (.clk(nor_5_out), .D(d_ff_25_q), .Q(d_ff_11_q), .preset(nor_6_out));  // open: Qn, en, reset
  D_Flip_Flop d_ff_12 (.clk(nor_5_out), .D(d_ff_26_q), .Q(d_ff_12_q), .preset(nor_6_out));  // open: Qn, en, reset
  D_Flip_Flop d_ff_13 (.clk(nor_5_out), .D(d_ff_27_q), .Q(d_ff_13_q), .preset(nor_6_out));  // open: Qn, en, reset
  D_Flip_Flop d_ff_14 (.clk(nor_5_out), .D(d_ff_28_q), .Q(d_ff_14_q), .preset(nor_6_out));  // open: Qn, en, reset
  D_Flip_Flop d_ff_15 (.clk(nor_5_out), .D(d_ff_29_q), .Q(d_ff_15_q), .preset(nor_6_out));  // open: Qn, en, reset
  D_Flip_Flop d_ff_16 (.clk(nor_5_out), .D(d_ff_30_q), .Q(d_ff_16_q), .preset(nor_6_out));  // open: Qn, en, reset
  D_Flip_Flop d_ff_17 (.clk(nor_5_out), .D(d_ff_31_q), .Q(d_ff_17_q), .preset(nor_6_out));  // open: Qn, en, reset
  D_Flip_Flop d_ff_18 (.clk(nor_5_out), .D(d_ff_32_q), .Q(d_ff_18_q), .preset(nor_6_out));  // open: Qn, en, reset
  D_Flip_Flop d_ff_19 (.clk(nor_5_out), .D(d_ff_33_q), .Q(d_ff_19_q), .preset(nor_6_out));  // open: Qn, en, reset
  D_Flip_Flop d_ff_20 (.clk(nor_5_out), .D(d_ff_34_q), .Q(d_ff_20_q), .preset(nor_6_out));  // open: Qn, en, reset
  D_Flip_Flop d_ff_21 (.clk(nor_5_out), .D(d_ff_35_q), .Q(d_ff_21_q), .preset(nor_6_out));  // open: Qn, en, reset
  D_Flip_Flop d_ff_22 (.clk(nor_5_out), .D(d_ff_36_q), .Q(d_ff_22_q), .preset(nor_6_out));  // open: Qn, en, reset
  nor nor_7 (nor_7_out, d_ff_6_q, d_ff_7_q);
  D_Flip_Flop d_ff_23 (.clk(nACLK), .D(d_ff_8_q), .Q(d_ff_23_q), .Qn(d_ff_23_qn));  // open: preset, en, reset
  D_Flip_Flop d_ff_24 (.clk(nACLK), .D(d_ff_9_q), .Q(d_ff_24_q), .Qn(d_ff_24_qn));  // open: preset, en, reset
  D_Flip_Flop d_ff_25 (.clk(nACLK), .D(d_ff_10_q), .Q(d_ff_25_q), .Qn(d_ff_25_qn));  // open: preset, en, reset
  D_Flip_Flop d_ff_26 (.clk(nACLK), .D(d_ff_11_q), .Q(d_ff_26_q), .Qn(d_ff_26_qn));  // open: preset, en, reset
  D_Flip_Flop d_ff_27 (.clk(nACLK), .D(d_ff_12_q), .Q(d_ff_27_q), .Qn(d_ff_27_qn));  // open: preset, en, reset
  D_Flip_Flop d_ff_28 (.clk(nACLK), .D(d_ff_13_q), .Q(d_ff_28_q), .Qn(d_ff_28_qn));  // open: preset, en, reset
  D_Flip_Flop d_ff_29 (.clk(nACLK), .D(d_ff_14_q), .Q(d_ff_29_q), .Qn(d_ff_29_qn));  // open: preset, en, reset
  D_Flip_Flop d_ff_30 (.clk(nACLK), .D(d_ff_15_q), .Q(d_ff_30_q), .Qn(d_ff_30_qn));  // open: preset, en, reset
  D_Flip_Flop d_ff_31 (.clk(nACLK), .D(d_ff_16_q), .Q(d_ff_31_q), .Qn(d_ff_31_qn));  // open: preset, en, reset
  D_Flip_Flop d_ff_32 (.clk(nACLK), .D(d_ff_17_q), .Q(d_ff_32_q), .Qn(d_ff_32_qn));  // open: preset, en, reset
  D_Flip_Flop d_ff_33 (.clk(nACLK), .D(d_ff_18_q), .Q(d_ff_33_q), .Qn(d_ff_33_qn));  // open: preset, en, reset
  D_Flip_Flop d_ff_34 (.clk(nACLK), .D(d_ff_19_q), .Q(d_ff_34_q), .Qn(d_ff_34_qn));  // open: preset, en, reset
  D_Flip_Flop d_ff_35 (.clk(nACLK), .D(d_ff_20_q), .Q(d_ff_35_q), .Qn(d_ff_35_qn));  // open: preset, en, reset
  D_Flip_Flop d_ff_36 (.clk(nACLK), .D(d_ff_21_q), .Q(d_ff_36_q), .Qn(d_ff_36_qn));  // open: preset, en, reset
  D_Flip_Flop d_ff_37 (.clk(nACLK), .D(d_ff_22_q), .Q(d_ff_37_q), .Qn(d_ff_37_qn));  // open: preset, en, reset
  and and_3 (and_3_out, Nor2_out, d_ff_1_qn);
  nor nor_8 (nor_8_out, PHI1, nR4015);
  nor nor_9 (nor_9_out, and_3_out, nor_10_out);
  nor nor_10 (nor_10_out, nor_9_out, d_ff_2_q, Res, nor_8_out);
  nor Nor1 (Nor1_out, d_ff_23_qn, d_ff_24_q, d_ff_25_qn, d_ff_26_q, d_ff_27_q, d_ff_28_q, d_ff_29_q, d_ff_30_qn, d_ff_31_qn, d_ff_32_q, d_ff_33_q, d_ff_34_q, d_ff_35_qn, d_ff_36_qn, d_ff_37_qn);
  nor Nor0 (out_14, d_ff_23_q, d_ff_24_q, d_ff_25_q, d_ff_26_q, d_ff_27_q, d_ff_28_q, d_ff_29_q, d_ff_30_q, d_ff_31_q, d_ff_32_q, d_ff_33_q, d_ff_34_q, d_ff_35_q, d_ff_36_q, d_ff_37_q);
  D_Flip_Flop d_ff_38 (.clk(nACLK), .D(nor_9_out), .Qn(d_ff_38_qn));  // open: Q, preset, en, reset
  not not_2 (not_2_out, nR4015);
  nor Nor2 (Nor2_out, d_ff_30_q, d_ff_23_qn, d_ff_24_qn, d_ff_25_qn, d_ff_26_qn, d_ff_27_qn, d_ff_28_q, d_ff_29_q, d_ff_31_q, d_ff_32_qn, d_ff_33_q, d_ff_34_qn, d_ff_35_q, d_ff_36_q, d_ff_37_q, d_ff_3_qn);
  assign D6_State = not_2_out ? ~d_ff_38_qn : 1'bz;  // Controlled_Inverter controlled_inverter_1
  nor Nor3 (Nor3_out, d_ff_23_qn, d_ff_24_qn, d_ff_25_q, d_ff_26_q, d_ff_27_qn, d_ff_28_q, d_ff_29_qn, d_ff_30_qn, d_ff_31_q, d_ff_32_q, d_ff_33_qn, d_ff_34_qn, d_ff_35_q, d_ff_36_qn, d_ff_37_q);
  nor Nor5 (Nor5_out, d_ff_23_qn, d_ff_24_q, d_ff_25_q, d_ff_26_q, d_ff_27_q, d_ff_28_qn, d_ff_29_qn, d_ff_30_q, d_ff_31_q, d_ff_32_q, d_ff_33_q, d_ff_34_q, d_ff_35_qn, d_ff_36_q, d_ff_37_q);
  nor Nor4 (Nor4_out, d_ff_23_qn, d_ff_24_qn, d_ff_25_q, d_ff_26_q, d_ff_27_q, d_ff_28_q, d_ff_29_q, d_ff_30_q, d_ff_31_q, d_ff_32_qn, d_ff_33_qn, d_ff_34_q, d_ff_35_qn, d_ff_36_qn, d_ff_37_q);
  nor nor_11 (nor_11_out, out_14, d_ff_37_q, d_ff_36_q);
  and and_4 (and_4_out, d_ff_37_q, d_ff_36_q);
  not not_3 (INT, nor_12_out);
  nor nor_12 (nor_12_out, nor_10_out, DMCINT);
  nor nor_13 (nor_13_out, nor_11_out, and_4_out);
  Counter #(.width(16), .max('hffff)) counter_1 (
    .Q(counter_1_q), .clk(nACLK), .clr(Nor5_out));  // open: load, D, count, carry
  nor nor_14 (nor_14_out, Nor5_out, Nor4_out, Nor3_out, Nor2_out, Nor1_out, nor_7_out);
  nor nor_15 (nor_15_out, Nor2_out, Nor4_out, Nor1_out, nor_7_out);
  Register #(.width(16)) register_1 (.D(counter_1_q), .clk(Nor5_out));  // open: en, Q, clr
  nor nor_16 (nor_16_out, ACLK, nor_14_out);
  nor nor_17 (nor_17_out, ACLK, nor_15_out);
  Counter #(.width(16), .max('hffff)) counter_2 (
    .Q(counter_2_q), .clk(nACLK), .clr(INT));  // open: load, D, count, carry
  Counter #(.width(16), .max('hffff)) counter_3 (
    .Q(counter_3_q), .clk(nACLK), .clr(not_4_out));  // open: load, D, count, carry
  not not_4 (not_4_out, nLFO2);
  not not_5 (nLFO1, nor_16_out);
  not not_6 (nLFO2, nor_17_out);
  Register #(.width(16)) register_2 (.D(counter_2_q), .clk(INT));  // open: en, Q, clr
  Register #(.width(16), .trigger("falling")) register_3 (
    .D(counter_3_q), .Q(register_3_q), .clk(nLFO2));  // open: en, clr
  // Probe on register_3_q
  Counter counter_4 (.clk(INT));  // open: load, D, count, Q, carry, clr
  Counter counter_5 (.clk(INT));  // open: load, D, count, Q, carry, clr
  Counter #(.width(15), .max('h7fff), .trigger("falling")) counter_6 (
    .clk(nLFO1), .clr(in_1));  // open: load, D, count, Q, carry
  Counter #(.width(15), .max('h7fff), .trigger("falling")) counter_7 (
    .clk(nLFO2), .clr(in_1));  // open: load, D, count, Q, carry

  // Notes on the sheet:
  //   NORFF1
  //   RS2
  //   NORFF2
  //   DL1
  //   DL3
  //   NOR6
  //   DL4
  //   NOR3
  //   INV1
  //   NOR1
  //   NOR2
  //   DL6
  //   DL5
  //   NOR7
  //   0
  //   1
  //   2
  //   3
  //   4
  //   5
  //   6
  //   7
  //   8
  //   9
  //   10
  //   11
  //   12
  //   13
  //   14
  //   AND
  //   RS1
  //   NOR4
  //   NORFF2
  //   NORFF1
  //   DL2
  //   Nor3=11185
  //   Nor2=14914
  //   Nor1=18640
  //   Nor5=3728
  //   Nor4=7456
  //   NOR5
  //   INV2
endmodule

module DLATCH (
  input  EN,
  input  in,
  output out,
  output nout
);

  D_Flip_Flop #(.trigger("high")) d_ff_1 (.clk(EN), .D(in), .Q(out), .Qn(nout));  // open: preset, en, reset
endmodule

module D_positive (
  input  EN,
  input  in,
  output out,
  output nout
);

  D_Flip_Flop d_ff_1 (.clk(EN), .D(in), .Q(out), .Qn(nout));  // open: preset, en, reset
endmodule

module Masterclock (
  input  PHI0,
  input  RES,
  output PHI1,
  output PHI2,
  output ACLK,
  output nACLK
);

  wire d_ff_1_qn, d_ff_2_qn, nor_1_out, nor_2_out, not_2_out;

  not not_1 (PHI1, PHI0);
  not not_2 (not_2_out, PHI1);
  D_Flip_Flop d_ff_1 (.clk(PHI1), .D(nor_1_out), .Qn(d_ff_1_qn));  // open: Q, preset, en, reset
  D_Flip_Flop d_ff_2 (.clk(PHI0), .D(d_ff_1_qn), .Qn(d_ff_2_qn));  // open: Q, preset, en, reset
  nor nor_1 (nor_1_out, d_ff_2_qn, RES);
  nor nor_2 (nor_2_out, nor_1_out, not_2_out);
  nor nor_3 (nACLK, not_2_out, PHI0, d_ff_2_qn);
  not not_3 (ACLK, nor_2_out);

  assign PHI2 = PHI0;

  // Notes on the sheet:
  //   INV1
  //   DL1
  //   DL2
  //   NOR1
  //   NOR2
  //   NOR3
endmodule
