// Logisim project Noiserev.circ as structural Verilog: 10 circuits, main circuit main
module main (
  input  D7,
  input  D6,
  input  D5,
  input  D4,
  input  D3,
  input  D2,
  input  D1,
  input  D0,
  input  W400E,
  input  W400F,
  input  W400C,
  input  Res,
  input  NORND,
  input  nLFO1,
  output PHI1,
  output PHI2,
  output ACLK,
  output nACLK,
  output out_19,
  output out_20,
  output out_21,
  output out_22
);

  wire and_1_out, and_2_out, clock_1_out, d_latch_1_q, d_latch_2_q, d_latch_3_q, d_latch_4_q, d_latch_5_q,
       d_latch_6_q, d_latch_7_q, d_latch_8_q, d_latch_9_q, d_latch_10_nq, envelope_control_1_eres,
       envelope_control_1_estep, envelope_control_1_load, envelope_control_1_output_oec,
       envelope_control_1_reload, envelope_control_1_step, envelope_frequency_divider_1_output,
       envelope_output_counter_1_env0, envelope_output_counter_1_env1, envelope_output_counter_1_env2,
       envelope_output_counter_1_env3, envelope_output_counter_1_output_oec, frequency_lfsr_1_fload,
       lfsr_1_rndout, multiplexer_1_out, multiplexer_2_out, multiplexer_3_out, multiplexer_4_out, not_1_out,
       not_2_out, not_3_out, not_4_out, not_5_out;
  wire [14:0] counter_1_q, register_1_q;

  Clock clock_1 (.out(clock_1_out));
  and and_1 (and_1_out, ACLK, W400E);
  D_latch d_latch_1 (.En(and_1_out), .In(D3), .Q(d_latch_1_q));  // open: nQ
  D_latch d_latch_2 (.En(and_1_out), .In(D2), .Q(d_latch_2_q));  // open: nQ
  D_latch d_latch_3 (.En(and_1_out), .In(D1), .Q(d_latch_3_q));  // open: nQ
  D_latch d_latch_4 (.En(and_1_out), .In(D0), .Q(d_latch_4_q));  // open: nQ
  and and_2 (and_2_out, ACLK, W400C);
  D_latch d_latch_5 (.En(and_2_out), .In(D0), .Q(d_latch_5_q));  // open: nQ
  D_latch d_latch_6 (.En(and_2_out), .In(D1), .Q(d_latch_6_q));  // open: nQ
  D_latch d_latch_7 (.En(and_2_out), .In(D2), .Q(d_latch_7_q));  // open: nQ
  D_latch d_latch_8 (.En(and_2_out), .In(D3), .Q(d_latch_8_q));  // open: nQ
  D_latch d_latch_9 (.En(and_2_out), .In(D4), .Q(d_latch_9_q));  // open: nQ
  D_latch d_latch_10 (.En(and_2_out), .In(D5), .nQ(d_latch_10_nq));  // open: Q
  Masterclock masterclock_1 (.PHI0(clock_1_out), .RES(Res), .PHI1(PHI1), .PHI2(PHI2), .ACLK(ACLK), .nACLK(nACLK));
  not not_1 (not_1_out, ACLK);
  Frequency_LFSR frequency_lfsr_1 (
    .FLOAD(frequency_lfsr_1_fload), .nACLK(nACLK), .nACLK1(not_1_out), .RES(Res), .F0(d_latch_4_q),
    .F1(d_latch_3_q), .F2(d_latch_2_q), .F3(d_latch_1_q));
  Counter #(.width(15), .max('h7fff)) counter_1 (
    .Q(counter_1_q), .clk(PHI1), .clr(frequency_lfsr_1_fload));  // open: load, D, count, carry
  // Probe on register_1_q
  Register #(.width(15)) register_1 (.D(counter_1_q), .Q(register_1_q), .clk(frequency_lfsr_1_fload));  // open: en, clr
  LFSR lfsr_1 (
    .RSTEP(frequency_lfsr_1_fload), .ACLK(ACLK), .W400E(W400E), .D7(D7), .NORND(NORND), .RNDOUT(lfsr_1_rndout));
  Envelope_frequency_divider envelope_frequency_divider_1 (
    .nACLK(nACLK), .Vol0(d_latch_5_q), .LOAD(envelope_control_1_load), .STEP(envelope_control_1_step),
    .RES(Res), .Vol1(d_latch_6_q), .Vol2(d_latch_7_q), .Vol3(d_latch_8_q),
    .Output(envelope_frequency_divider_1_output));
  Envelope_output_counter envelope_output_counter_1 (
    .nACLK(nACLK), .Input_OEC(envelope_control_1_output_oec), .Eres(envelope_control_1_eres),
    .Estep(envelope_control_1_estep), .RES(Res), .Reload(envelope_control_1_reload),
    .Env0(envelope_output_counter_1_env0), .Env1(envelope_output_counter_1_env1),
    .Env2(envelope_output_counter_1_env2), .Env3(envelope_output_counter_1_env3),
    .Output_OEC(envelope_output_counter_1_output_oec));
  Envelope_Control envelope_control_1 (
    .nACLK(nACLK), .nLFO1(nLFO1), .W400F(W400F), .Input_ERC(envelope_frequency_divider_1_output),
    .Input_OEC(envelope_output_counter_1_output_oec), .RND_LC(d_latch_10_nq),
    .RELOAD(envelope_control_1_reload), .LOAD(envelope_control_1_load), .STEP(envelope_control_1_step),
    .Estep(envelope_control_1_estep), .Eres(envelope_control_1_eres),
    .Output_OEC(envelope_control_1_output_oec));
  Multiplexer multiplexer_1 (
    .in0(envelope_output_counter_1_env0), .in1(d_latch_5_q), .out(multiplexer_1_out), .sel(d_latch_9_q));  // open: en
  not not_2 (not_2_out, multiplexer_1_out);
  not not_3 (not_3_out, multiplexer_2_out);
  Multiplexer multiplexer_2 (
    .in0(envelope_output_counter_1_env1), .in1(d_latch_6_q), .out(multiplexer_2_out), .sel(d_latch_9_q));  // open: en
  not not_4 (not_4_out, multiplexer_3_out);
  Multiplexer multiplexer_3 (
    .in0(envelope_output_counter_1_env2), .in1(d_latch_7_q), .out(multiplexer_3_out), .sel(d_latch_9_q));  // open: en
  Multiplexer multiplexer_4 (
    .in0(envelope_output_counter_1_env3), .in1(d_latch_8_q), .out(multiplexer_4_out), .sel(d_latch_9_q));  // open: en
  not not_5 (not_5_out, multiplexer_4_out);
  nor nor_1 (out_19, not_2_out, lfsr_1_rndout);
  nor nor_2 (out_20, not_3_out, lfsr_1_rndout);
  nor nor_3 (out_21, not_4_out, lfsr_1_rndout);
  nor nor_4 (out_22, not_5_out, lfsr_1_rndout);

  // Notes on the sheet:
  //   F3
  //   F2
  //   F1
  //   F0
  //   Vol0
  //   Vol1
  //   Vol2
  //   Vol3
endmodule

module Table (
  input  F3,
  input  F2,
  input  F1,
  input  F0,
  output LP0,
  output LP1,
  output LP2,
  output LP3,
  output LP4,
  output LP5,
  output LP6,
  output LP7,
  output LP8,
  output LP9,
  output LP10
);

  wire not_1_out, not_2_out, not_3_out, not_4_out, transistor_19_out, transistor_29_out, transistor_30_out,
       transistor_44_out, transistor_62_out, transistor_74_out, transistor_75_out, transistor_88_out,
       transistor_98_out, transistor_114_out, transistor_124_out, transistor_125_out, transistor_136_out,
       transistor_156_out, transistor_170_out, transistor_171_out;

  not not_1 (not_1_out, F3);
  not not_2 (not_2_out, F2);
  not not_3 (not_3_out, F1);
  not not_4 (not_4_out, F0);
  Transistor #(.\type ("n"), .gate("br")) transistor_1 (.in(1'b0), .out(LP0), .gate(transistor_29_out));
  Transistor #(.\type ("n"), .gate("br")) transistor_2 (.in(1'b0), .out(LP0), .gate(transistor_19_out));
  Transistor #(.\type ("n"), .gate("br")) transistor_3 (.in(1'b0), .out(LP1), .gate(transistor_19_out));
  Transistor #(.\type ("n"), .gate("br")) transistor_4 (.in(1'b0), .out(LP3), .gate(transistor_29_out));
  Transistor #(.\type ("n"), .gate("br")) transistor_5 (.in(1'b0), .out(LP3), .gate(transistor_19_out));
  Transistor #(.\type ("n"), .gate("br")) transistor_6 (.in(1'b0), .out(LP4), .gate(transistor_29_out));
  Transistor #(.\type ("n"), .gate("br")) transistor_7 (.in(1'b0), .out(LP5), .gate(transistor_29_out));
  Transistor #(.\type ("n"), .gate("br")) transistor_8 (.in(1'b0), .out(LP5), .gate(transistor_19_out));
  Transistor #(.\type ("n"), .gate("br")) transistor_9 (.in(1'b0), .out(LP6), .gate(transistor_19_out));
  Transistor #(.\type ("n"), .gate("br")) transistor_10 (.in(1'b0), .out(LP6), .gate(transistor_29_out));
  Transistor #(.\type ("n"), .gate("br")) transistor_11 (.in(1'b0), .out(LP7), .gate(transistor_29_out));
  Transistor #(.\type ("n"), .gate("br")) transistor_12 (.in(1'b0), .out(LP7), .gate(transistor_19_out));
  Transistor #(.\type ("n"), .gate("br")) transistor_13 (.in(1'b0), .out(LP8), .gate(transistor_29_out));
  Transistor #(.\type ("n"), .gate("br")) transistor_14 (.in(1'b0), .out(LP8), .gate(transistor_19_out));
  Transistor #(.\type ("n"), .gate("br")) transistor_15 (.in(1'b0), .out(LP9), .gate(transistor_19_out));
  Transistor #(.\type ("n"), .gate("br")) transistor_16 (.in(1'b0), .out(LP9), .gate(transistor_29_out));
  Transistor #(.\type ("n"), .gate("br")) transistor_17 (.in(1'b0), .out(LP10), .gate(transistor_29_out));
  Transistor #(.\type ("n"), .gate("br")) transistor_18 (.in(1'b0), .out(LP10), .gate(transistor_19_out));
  Transistor #(.\type ("n")) transistor_19 (.in(1'b0), .out(transistor_19_out), .gate(not_1_out));
  Transistor #(.\type ("n")) transistor_20 (.in(1'b0), .out(transistor_19_out), .gate(not_2_out));
  Transistor #(.\type ("n")) transistor_21 (.in(1'b0), .out(transistor_19_out), .gate(not_3_out));
  Transistor #(.\type ("n")) transistor_22 (.in(1'b0), .out(transistor_19_out), .gate(not_4_out));
  Pull_Resistor #(.pull(1)) pull_resistor_1 (.node(transistor_19_out));
  Transistor #(.\type ("n"), .gate("br")) transistor_23 (.in(1'b0), .out(LP0), .gate(transistor_30_out));
  Transistor #(.\type ("n"), .gate("br")) transistor_24 (.in(1'b0), .out(LP2), .gate(transistor_30_out));
  Transistor #(.\type ("n"), .gate("br")) transistor_25 (.in(1'b0), .out(LP3), .gate(transistor_30_out));
  Transistor #(.\type ("n"), .gate("br")) transistor_26 (.in(1'b0), .out(LP4), .gate(transistor_30_out));
  Transistor #(.\type ("n"), .gate("br")) transistor_27 (.in(1'b0), .out(LP5), .gate(transistor_30_out));
  Transistor #(.\type ("n"), .gate("br")) transistor_28 (.in(1'b0), .out(LP6), .gate(transistor_30_out));
  Transistor #(.\type ("n")) transistor_29 (.in(1'b0), .out(transistor_29_out), .gate(not_1_out));
  Transistor #(.\type ("n")) transistor_30 (.in(1'b0), .out(transistor_30_out), .gate(not_1_out));
  Transistor #(.\type ("n")) transistor_31 (.in(1'b0), .out(transistor_29_out), .gate(not_2_out));
  Transistor #(.\type ("n")) transistor_32 (.in(1'b0), .out(transistor_30_out), .gate(not_2_out));
  Transistor #(.\type ("n")) transistor_33 (.in(1'b0), .out(transistor_30_out), .gate(F1));
  Transistor #(.\type ("n")) transistor_34 (.in(1'b0), .out(transistor_29_out), .gate(not_3_out));
  Transistor #(.\type ("n")) transistor_35 (.in(1'b0), .out(transistor_29_out), .gate(F0));
  Transistor #(.\type ("n")) transistor_36 (.in(1'b0), .out(transistor_30_out), .gate(not_4_out));
  Pull_Resistor #(.pull(1)) pull_resistor_2 (.node(transistor_29_out));
  Pull_Resistor #(.pull(1)) pull_resistor_3 (.node(transistor_30_out));
  Transistor #(.\type ("n"), .gate("br")) transistor_37 (.in(1'b0), .out(LP2), .gate(transistor_44_out));
  Transistor #(.\type ("n"), .gate("br")) transistor_38 (.in(1'b0), .out(LP3), .gate(transistor_44_out));
  Transistor #(.\type ("n"), .gate("br")) transistor_39 (.in(1'b0), .out(LP5), .gate(transistor_44_out));
  Transistor #(.\type ("n"), .gate("br")) transistor_40 (.in(1'b0), .out(LP6), .gate(transistor_44_out));
  Transistor #(.\type ("n"), .gate("br")) transistor_41 (.in(1'b0), .out(LP7), .gate(transistor_44_out));
  Transistor #(.\type ("n"), .gate("br")) transistor_42 (.in(1'b0), .out(LP8), .gate(transistor_44_out));
  Transistor #(.\type ("n"), .gate("br")) transistor_43 (.in(1'b0), .out(LP10), .gate(transistor_44_out));
  Transistor #(.\type ("n")) transistor_44 (.in(1'b0), .out(transistor_44_out), .gate(not_1_out));
  Transistor #(.\type ("n")) transistor_45 (.in(1'b0), .out(transistor_44_out), .gate(not_2_out));
  Transistor #(.\type ("n")) transistor_46 (.in(1'b0), .out(transistor_44_out), .gate(F1));
  Transistor #(.\type ("n")) transistor_47 (.in(1'b0), .out(transistor_44_out), .gate(F0));
  Pull_Resistor #(.pull(1)) pull_resistor_4 (.node(transistor_44_out));
  Transistor #(.\type ("n"), .gate("br")) transistor_48 (.in(1'b0), .out(LP0), .gate(transistor_62_out));
  Transistor #(.\type ("n"), .gate("br")) transistor_49 (.in(1'b0), .out(LP0), .gate(transistor_74_out));
  Transistor #(.\type ("n"), .gate("br")) transistor_50 (.in(1'b0), .out(LP1), .gate(transistor_62_out));
  Transistor #(.\type ("n"), .gate("br")) transistor_51 (.in(1'b0), .out(LP2), .gate(transistor_74_out));
  Transistor #(.\type ("n"), .gate("br")) transistor_52 (.in(1'b0), .out(LP2), .gate(transistor_62_out));
  Transistor #(.\type ("n"), .gate("br")) transistor_53 (.in(1'b0), .out(LP3), .gate(transistor_62_out));
  Transistor #(.\type ("n"), .gate("br")) transistor_54 (.in(1'b0), .out(LP3), .gate(transistor_74_out));
  Transistor #(.\type ("n"), .gate("br")) transistor_55 (.in(1'b0), .out(LP4), .gate(transistor_74_out));
  Transistor #(.\type ("n"), .gate("br")) transistor_56 (.in(1'b0), .out(LP6), .gate(transistor_74_out));
  Transistor #(.\type ("n"), .gate("br")) transistor_57 (.in(1'b0), .out(LP6), .gate(transistor_62_out));
  Transistor #(.\type ("n"), .gate("br")) transistor_58 (.in(1'b0), .out(LP7), .gate(transistor_74_out));
  Transistor #(.\type ("n"), .gate("br")) transistor_59 (.in(1'b0), .out(LP7), .gate(transistor_62_out));
  Transistor #(.\type ("n"), .gate("br")) transistor_60 (.in(1'b0), .out(LP8), .gate(transistor_62_out));
  Transistor #(.\type ("n"), .gate("br")) transistor_61 (.in(1'b0), .out(LP10), .gate(transistor_62_out));
  Transistor #(.\type ("n")) transistor_62 (.in(1'b0), .out(transistor_62_out), .gate(not_1_out));
  Transistor #(.\type ("n")) transistor_63 (.in(1'b0), .out(transistor_62_out), .gate(F2));
  Transistor #(.\type ("n")) transistor_64 (.in(1'b0), .out(transistor_62_out), .gate(not_3_out));
  Transistor #(.\type ("n")) transistor_65 (.in(1'b0), .out(transistor_62_out), .gate(not_4_out));
  Pull_Resistor #(.pull(1)) pull_resistor_5 (.node(transistor_62_out));
  Transistor #(.\type ("n"), .gate("br")) transistor_66 (.in(1'b0), .out(LP0), .gate(transistor_75_out));
  Transistor #(.\type ("n"), .gate("br")) transistor_67 (.in(1'b0), .out(LP1), .gate(transistor_75_out));
  Transistor #(.\type ("n"), .gate("br")) transistor_68 (.in(1'b0), .out(LP3), .gate(transistor_75_out));
  Transistor #(.\type ("n"), .gate("br")) transistor_69 (.in(1'b0), .out(LP4), .gate(transistor_75_out));
  Transistor #(.\type ("n"), .gate("br")) transistor_70 (.in(1'b0), .out(LP5), .gate(transistor_75_out));
  Transistor #(.\type ("n"), .gate("br")) transistor_71 (.in(1'b0), .out(LP6), .gate(transistor_75_out));
  Transistor #(.\type ("n"), .gate("br")) transistor_72 (.in(1'b0), .out(LP7), .gate(transistor_75_out));
  Transistor #(.\type ("n"), .gate("br")) transistor_73 (.in(1'b0), .out(LP10), .gate(transistor_75_out));
  Transistor #(.\type ("n")) transistor_74 (.in(1'b0), .out(transistor_74_out), .gate(not_1_out));
  Transistor #(.\type ("n")) transistor_75 (.in(1'b0), .out(transistor_75_out), .gate(not_1_out));
  Transistor #(.\type ("n")) transistor_76 (.in(1'b0), .out(transistor_74_out), .gate(F2));
  Transistor #(.\type ("n")) transistor_77 (.in(1'b0), .out(transistor_75_out), .gate(F2));
  Transistor #(.\type ("n")) transistor_78 (.in(1'b0), .out(transistor_75_out), .gate(F1));
  Transistor #(.\type ("n")) transistor_79 (.in(1'b0), .out(transistor_74_out), .gate(not_3_out));
  Transistor #(.\type ("n")) transistor_80 (.in(1'b0), .out(transistor_74_out), .gate(F0));
  Transistor #(.\type ("n")) transistor_81 (.in(1'b0), .out(transistor_75_out), .gate(not_4_out));
  Pull_Resistor #(.pull(1)) pull_resistor_6 (.node(transistor_74_out));
  Pull_Resistor #(.pull(1)) pull_resistor_7 (.node(transistor_75_out));
  Transistor #(.\type ("n"), .gate("br")) transistor_82 (.in(1'b0), .out(LP0), .gate(transistor_88_out));
  Transistor #(.\type ("n"), .gate("br")) transistor_83 (.in(1'b0), .out(LP1), .gate(transistor_88_out));
  Transistor #(.\type ("n"), .gate("br")) transistor_84 (.in(1'b0), .out(LP4), .gate(transistor_88_out));
  Transistor #(.\type ("n"), .gate("br")) transistor_85 (.in(1'b0), .out(LP6), .gate(transistor_88_out));
  Transistor #(.\type ("n"), .gate("br")) transistor_86 (.in(1'b0), .out(LP8), .gate(transistor_88_out));
  Transistor #(.\type ("n"), .gate("br")) transistor_87 (.in(1'b0), .out(LP9), .gate(transistor_88_out));
  Transistor #(.\type ("n")) transistor_88 (.in(1'b0), .out(transistor_88_out), .gate(not_1_out));
  Transistor #(.\type ("n")) transistor_89 (.in(1'b0), .out(transistor_88_out), .gate(F2));
  Transistor #(.\type ("n")) transistor_90 (.in(1'b0), .out(transistor_88_out), .gate(F1));
  Transistor #(.\type ("n")) transistor_91 (.in(1'b0), .out(transistor_88_out), .gate(F0));
  Pull_Resistor #(.pull(1)) pull_resistor_8 (.node(transistor_88_out));
  Transistor #(.\type ("n"), .gate("br")) transistor_92 (.in(1'b0), .out(LP0), .gate(transistor_98_out));
  Transistor #(.\type ("n"), .gate("br")) transistor_93 (.in(1'b0), .out(LP1), .gate(transistor_98_out));
  Transistor #(.\type ("n"), .gate("br")) transistor_94 (.in(1'b0), .out(LP2), .gate(transistor_98_out));
  Transistor #(.\type ("n"), .gate("br")) transistor_95 (.in(1'b0), .out(LP3), .gate(transistor_98_out));
  Transistor #(.\type ("n"), .gate("br")) transistor_96 (.in(1'b0), .out(LP6), .gate(transistor_98_out));
  Transistor #(.\type ("n"), .gate("br")) transistor_97 (.in(1'b0), .out(LP7), .gate(transistor_98_out));
  Transistor #(.\type ("n")) transistor_98 (.in(1'b0), .out(transistor_98_out), .gate(F3));
  Transistor #(.\type ("n")) transistor_99 (.in(1'b0), .out(transistor_98_out), .gate(not_2_out));
  Transistor #(.\type ("n")) transistor_100 (.in(1'b0), .out(transistor_98_out), .gate(not_3_out));
  Transistor #(.\type ("n")) transistor_101 (.in(1'b0), .out(transistor_98_out), .gate(not_4_out));
  Pull_Resistor #(.pull(1)) pull_resistor_9 (.node(transistor_98_out));
  Transistor #(.\type ("n"), .gate("br")) transistor_102 (.in(1'b0), .out(LP0), .gate(transistor_125_out));
  Transistor #(.\type ("n"), .gate("br")) transistor_103 (.in(1'b0), .out(LP0), .gate(transistor_114_out));
  Transistor #(.\type ("n"), .gate("br")) transistor_104 (.in(1'b0), .out(LP1), .gate(transistor_114_out));
  Transistor #(.\type ("n"), .gate("br")) transistor_105 (.in(1'b0), .out(LP1), .gate(transistor_125_out));
  Transistor #(.\type ("n"), .gate("br")) transistor_106 (.in(1'b0), .out(LP2), .gate(transistor_114_out));
  Transistor #(.\type ("n"), .gate("br")) transistor_107 (.in(1'b0), .out(LP3), .gate(transistor_125_out));
  Transistor #(.\type ("n"), .gate("br")) transistor_108 (.in(1'b0), .out(LP3), .gate(transistor_114_out));
  Transistor #(.\type ("n"), .gate("br")) transistor_109 (.in(1'b0), .out(LP6), .gate(transistor_114_out));
  Transistor #(.\type ("n"), .gate("br")) transistor_110 (.in(1'b0), .out(LP7), .gate(transistor_125_out));
  Transistor #(.\type ("n"), .gate("br")) transistor_111 (.in(1'b0), .out(LP7), .gate(transistor_114_out));
  Transistor #(.\type ("n"), .gate("br")) transistor_112 (.in(1'b0), .out(LP8), .gate(transistor_125_out));
  Transistor #(.\type ("n"), .gate("br")) transistor_113 (.in(1'b0), .out(LP8), .gate(transistor_114_out));
  Transistor #(.\type ("n")) transistor_114 (.in(1'b0), .out(transistor_114_out), .gate(F3));
  Transistor #(.\type ("n")) transistor_115 (.in(1'b0), .out(transistor_114_out), .gate(not_2_out));
  Transistor #(.\type ("n")) transistor_116 (.in(1'b0), .out(transistor_114_out), .gate(not_3_out));
  Transistor #(.\type ("n")) transistor_117 (.in(1'b0), .out(transistor_114_out), .gate(F0));
  Pull_Resistor #(.pull(1)) pull_resistor_10 (.node(transistor_114_out));
  Transistor #(.\type ("n"), .gate("br")) transistor_118 (.in(1'b0), .out(LP0), .gate(transistor_124_out));
  Transistor #(.\type ("n"), .gate("br")) transistor_119 (.in(1'b0), .out(LP1), .gate(transistor_124_out));
  Transistor #(.\type ("n"), .gate("br")) transistor_120 (.in(1'b0), .out(LP3), .gate(transistor_124_out));
  Transistor #(.\type ("n"), .gate("br")) transistor_121 (.in(1'b0), .out(LP4), .gate(transistor_124_out));
  Transistor #(.\type ("n"), .gate("br")) transistor_122 (.in(1'b0), .out(LP8), .gate(transistor_124_out));
  Transistor #(.\type ("n"), .gate("br")) transistor_123 (.in(1'b0), .out(LP9), .gate(transistor_124_out));
  Transistor #(.\type ("n")) transistor_124 (.in(1'b0), .out(transistor_124_out), .gate(F3));
  Transistor #(.\type ("n")) transistor_125 (.in(1'b0), .out(transistor_125_out), .gate(F3));
  Transistor #(.\type ("n")) transistor_126 (.in(1'b0), .out(transistor_125_out), .gate(not_2_out));
  Transistor #(.\type ("n")) transistor_127 (.in(1'b0), .out(transistor_124_out), .gate(not_2_out));
  Transistor #(.\type ("n")) transistor_128 (.in(1'b0), .out(transistor_125_out), .gate(F1));
  Transistor #(.\type ("n")) transistor_129 (.in(1'b0), .out(transistor_124_out), .gate(F1));
  Transistor #(.\type ("n")) transistor_130 (.in(1'b0), .out(transistor_124_out), .gate(F0));
  Transistor #(.\type ("n")) transistor_131 (.in(1'b0), .out(transistor_125_out), .gate(not_4_out));
  Pull_Resistor #(.pull(1)) pull_resistor_11 (.node(transistor_125_out));
  Pull_Resistor #(.pull(1)) pull_resistor_12 (.node(transistor_124_out));
  Transistor #(.\type ("n"), .gate("br")) transistor_132 (.in(1'b0), .out(LP0), .gate(transistor_136_out));
  Transistor #(.\type ("n"), .gate("br")) transistor_133 (.in(1'b0), .out(LP2), .gate(transistor_136_out));
  Transistor #(.\type ("n"), .gate("br")) transistor_134 (.in(1'b0), .out(LP4), .gate(transistor_136_out));
  Transistor #(.\type ("n"), .gate("br")) transistor_135 (.in(1'b0), .out(LP8), .gate(transistor_136_out));
  Transistor #(.\type ("n")) transistor_136 (.in(1'b0), .out(transistor_136_out), .gate(F3));
  Transistor #(.\type ("n")) transistor_137 (.in(1'b0), .out(transistor_136_out), .gate(F2));
  Transistor #(.\type ("n")) transistor_138 (.in(1'b0), .out(transistor_136_out), .gate(not_3_out));
  Transistor #(.\type ("n")) transistor_139 (.in(1'b0), .out(transistor_136_out), .gate(not_4_out));
  Pull_Resistor #(.pull(1)) pull_resistor_13 (.node(transistor_136_out));
  Transistor #(.\type ("n"), .gate("br")) transistor_140 (.in(1'b0), .out(LP0), .gate(transistor_171_out));
  Transistor #(.\type ("n"), .gate("br")) transistor_141 (.in(1'b0), .out(LP0), .gate(transistor_156_out));
  Transistor #(.\type ("n"), .gate("br")) transistor_142 (.in(1'b0), .out(LP1), .gate(transistor_171_out));
  Transistor #(.\type ("n"), .gate("br")) transistor_143 (.in(1'b0), .out(LP1), .gate(transistor_156_out));
  Transistor #(.\type ("n"), .gate("br")) transistor_144 (.in(1'b0), .out(LP2), .gate(transistor_156_out));
  Transistor #(.\type ("n"), .gate("br")) transistor_145 (.in(1'b0), .out(LP2), .gate(transistor_171_out));
  Transistor #(.\type ("n"), .gate("br")) transistor_146 (.in(1'b0), .out(LP3), .gate(transistor_171_out));
  Transistor #(.\type ("n"), .gate("br")) transistor_147 (.in(1'b0), .out(LP4), .gate(transistor_171_out));
  Transistor #(.\type ("n"), .gate("br")) transistor_148 (.in(1'b0), .out(LP4), .gate(transistor_156_out));
  Transistor #(.\type ("n"), .gate("br")) transistor_149 (.in(1'b0), .out(LP5), .gate(transistor_171_out));
  Transistor #(.\type ("n"), .gate("br")) transistor_150 (.in(1'b0), .out(LP6), .gate(transistor_171_out));
  Transistor #(.\type ("n"), .gate("br")) transistor_151 (.in(1'b0), .out(LP6), .gate(transistor_156_out));
  Transistor #(.\type ("n"), .gate("br")) transistor_152 (.in(1'b0), .out(LP8), .gate(transistor_171_out));
  Transistor #(.\type ("n"), .gate("br")) transistor_153 (.in(1'b0), .out(LP8), .gate(transistor_156_out));
  Transistor #(.\type ("n"), .gate("br")) transistor_154 (.in(1'b0), .out(LP10), .gate(transistor_171_out));
  Transistor #(.\type ("n"), .gate("br")) transistor_155 (.in(1'b0), .out(LP10), .gate(transistor_156_out));
  Transistor #(.\type ("n")) transistor_156 (.in(1'b0), .out(transistor_156_out), .gate(F3));
  Transistor #(.\type ("n")) transistor_157 (.in(1'b0), .out(transistor_156_out), .gate(F2));
  Transistor #(.\type ("n")) transistor_158 (.in(1'b0), .out(transistor_156_out), .gate(not_3_out));
  Transistor #(.\type ("n")) transistor_159 (.in(1'b0), .out(transistor_156_out), .gate(F0));
  Pull_Resistor #(.pull(1)) pull_resistor_14 (.node(transistor_156_out));
  Transistor #(.\type ("n"), .gate("br")) transistor_160 (.in(1'b0), .out(LP0), .gate(transistor_170_out));
  Transistor #(.\type ("n"), .gate("br")) transistor_161 (.in(1'b0), .out(LP1), .gate(transistor_170_out));
  Transistor #(.\type ("n"), .gate("br")) transistor_162 (.in(1'b0), .out(LP2), .gate(transistor_170_out));
  Transistor #(.\type ("n"), .gate("br")) transistor_163 (.in(1'b0), .out(LP3), .gate(transistor_170_out));
  Transistor #(.\type ("n"), .gate("br")) transistor_164 (.in(1'b0), .out(LP4), .gate(transistor_170_out));
  Transistor #(.\type ("n"), .gate("br")) transistor_165 (.in(1'b0), .out(LP5), .gate(transistor_170_out));
  Transistor #(.\type ("n"), .gate("br")) transistor_166 (.in(1'b0), .out(LP6), .gate(transistor_170_out));
  Transistor #(.\type ("n"), .gate("br")) transistor_167 (.in(1'b0), .out(LP7), .gate(transistor_170_out));
  Transistor #(.\type ("n"), .gate("br")) transistor_168 (.in(1'b0), .out(LP8), .gate(transistor_170_out));
  Transistor #(.\type ("n"), .gate("br")) transistor_169 (.in(1'b0), .out(LP10), .gate(transistor_170_out));
  Transistor #(.\type ("n")) transistor_170 (.in(1'b0), .out(transistor_170_out), .gate(F3));
  Transistor #(.\type ("n")) transistor_171 (.in(1'b0), .out(transistor_171_out), .gate(F3));
  Transistor #(.\type ("n")) transistor_172 (.in(1'b0), .out(transistor_170_out), .gate(F2));
  Transistor #(.\type ("n")) transistor_173 (.in(1'b0), .out(transistor_171_out), .gate(F2));
  Transistor #(.\type ("n")) transistor_174 (.in(1'b0), .out(transistor_170_out), .gate(F1));
  Transistor #(.\type ("n")) transistor_175 (.in(1'b0), .out(transistor_171_out), .gate(F1));
  Transistor #(.\type ("n")) transistor_176 (.in(1'b0), .out(transistor_170_out), .gate(F0));
  Transistor #(.\type ("n")) transistor_177 (.in(1'b0), .out(transistor_171_out), .gate(not_4_out));
  Pull_Resistor #(.pull(1)) pull_resistor_15 (.node(transistor_171_out));
  Pull_Resistor #(.pull(1)) pull_resistor_16 (.node(transistor_170_out));
  Pull_Resistor #(.pull(1)) pull_resistor_17 (.node(LP0));
  Pull_Resistor #(.pull(1)) pull_resistor_18 (.node(LP1));
  Pull_Resistor #(.pull(1)) pull_resistor_19 (.node(LP2));
  Pull_Resistor #(.pull(1)) pull_resistor_20 (.node(LP3));
  Pull_Resistor #(.pull(1)) pull_resistor_21 (.node(LP4));
  Pull_Resistor #(.pull(1)) pull_resistor_22 (.node(LP5));
  Pull_Resistor #(.pull(1)) pull_resistor_23 (.node(LP6));
  Pull_Resistor #(.pull(1)) pull_resistor_24 (.node(LP7));
  Pull_Resistor #(.pull(1)) pull_resistor_25 (.node(LP8));
  Pull_Resistor #(.pull(1)) pull_resistor_26 (.node(LP9));
  Pull_Resistor #(.pull(1)) pull_resistor_27 (.node(LP10));
endmodule

module D_latch (
  input  En,
  input  In,
  output Q,
  output nQ
);

  D_Flip_Flop #(.trigger("high")) d_ff_1 (.clk(En), .D(In), .Q(Q), .Qn(nQ));  // open: preset, en, reset
endmodule

module Dpos (
  input  Clk,
  input  In,
  output Q,
  output nQ
);

  D_Flip_Flop d_ff_1 (.clk(Clk), .D(In), .Q(Q), .Qn(nQ));  // open: preset, en, reset
endmodule

module Frequency_LFSR (
  input  nACLK,
  input  nACLK1,
  input  RES,
  input  F0,
  input  F1,
  input  F2,
  input  F3,
  output FLOAD
);

  wire and_1_out, and_2_out, and_3_out, and_4_out, and_5_out, and_6_out, and_7_out, and_8_out, and_9_out,
       and_10_out, and_11_out, and_12_out, and_13_out, and_14_out, and_15_out, and_16_out, and_17_out,
       and_18_out, and_19_out, and_20_out, and_21_out, and_22_out, and_23_out, d_ff_1_qn, d_ff_2_qn,
       d_ff_3_qn, d_ff_4_qn, d_ff_5_qn, d_ff_6_qn, d_ff_7_qn, d_ff_8_qn, d_ff_9_qn, d_ff_10_qn, d_ff_11_qn,
       d_ff_12_qn, d_ff_13_qn, d_ff_14_qn, d_ff_15_qn, d_ff_16_qn, d_ff_17_qn, d_ff_18_qn, d_ff_19_qn,
       d_ff_20_qn, d_ff_21_qn, d_ff_22_qn, nor_1_out, nor_3_out, nor_4_out, nor_5_out, nor_6_out, nor_7_out,
       not_1_out, not_2_out, not_3_out, not_4_out, not_5_out, not_6_out, not_7_out, not_8_out, not_9_out,
       not_10_out, not_11_out, not_12_out, not_13_out, not_14_out, not_15_out, table_1_lp0, table_1_lp1,
       table_1_lp2, table_1_lp3, table_1_lp4, table_1_lp5, table_1_lp6, table_1_lp7, table_1_lp8,
       table_1_lp9, table_1_lp10;

  Table table_1 (
    .LP0(table_1_lp0), .LP1(table_1_lp1), .LP2(table_1_lp2), .LP3(table_1_lp3), .LP4(table_1_lp4),
    .LP5(table_1_lp5), .LP6(table_1_lp6), .LP7(table_1_lp7), .LP8(table_1_lp8), .LP9(table_1_lp9),
    .LP10(table_1_lp10), .F3(F3), .F2(F2), .F1(F1), .F0(F0));
  not not_1 (not_1_out, nACLK1);
  nor nor_1 (nor_1_out, not_1_out, nor_5_out);
  nor nor_2 (FLOAD, not_1_out, not_13_out);
  nor nor_3 (nor_3_out, nor_6_out, d_ff_22_qn, d_ff_20_qn);
  and and_1 (and_1_out, d_ff_22_qn, d_ff_20_qn);
  not not_2 (not_2_out, table_1_lp0);
  not not_3 (not_3_out, table_1_lp1);
  not not_4 (not_4_out, table_1_lp2);
  not not_5 (not_5_out, table_1_lp3);
  not not_6 (not_6_out, table_1_lp4);
  not not_7 (not_7_out, table_1_lp5);
  not not_8 (not_8_out, table_1_lp6);
  not not_9 (not_9_out, table_1_lp7);
  not not_10 (not_10_out, table_1_lp8);
  not not_11 (not_11_out, table_1_lp9);
  not not_12 (not_12_out, table_1_lp10);
  nor nor_4 (nor_4_out, nor_3_out, RES, and_1_out);
  and and_2 (and_2_out, FLOAD, table_1_lp0);
  and and_3 (and_3_out, FLOAD, not_2_out);
  and and_4 (and_4_out, FLOAD, table_1_lp1);
  and and_5 (and_5_out, FLOAD, not_3_out);
  and and_6 (and_6_out, FLOAD, table_1_lp2);
  and and_7 (and_7_out, FLOAD, not_4_out);
  and and_8 (and_8_out, FLOAD, table_1_lp3);
  and and_9 (and_9_out, FLOAD, not_5_out);
  and and_10 (and_10_out, FLOAD, table_1_lp4);
  and and_11 (and_11_out, FLOAD, not_6_out);
  and and_12 (and_12_out, FLOAD, table_1_lp5);
  and and_13 (and_13_out, FLOAD, not_7_out);
  and and_14 (and_14_out, FLOAD, table_1_lp6);
  and and_15 (and_15_out, FLOAD, not_8_out);
  and and_16 (and_16_out, FLOAD, table_1_lp7);
  and and_17 (and_17_out, FLOAD, not_9_out);
  and and_18 (and_18_out, FLOAD, table_1_lp8);
  and and_19 (and_19_out, FLOAD, not_10_out);
  and and_20 (and_20_out, FLOAD, table_1_lp9);
  and and_21 (and_21_out, FLOAD, not_11_out);
  and and_22 (and_22_out, FLOAD, table_1_lp10);
  and and_23 (and_23_out, FLOAD, not_12_out);
  D_Flip_Flop d_ff_1 (
    .clk(nor_1_out), .D(nor_4_out), .Qn(d_ff_1_qn), .preset(and_2_out), .reset(and_3_out));  // open: Q, en
  D_Flip_Flop d_ff_2 (
    .clk(nor_1_out), .D(d_ff_12_qn), .Qn(d_ff_2_qn), .preset(and_4_out), .reset(and_5_out));  // open: Q, en
  D_Flip_Flop d_ff_3 (
    .clk(nor_1_out), .D(d_ff_13_qn), .Qn(d_ff_3_qn), .preset(and_6_out), .reset(and_7_out));  // open: Q, en
  D_Flip_Flop d_ff_4 (
    .clk(nor_1_out), .D(d_ff_14_qn), .Qn(d_ff_4_qn), .preset(and_8_out), .reset(and_9_out));  // open: Q, en
  D_Flip_Flop d_ff_5 (
    .clk(nor_1_out), .D(d_ff_15_qn), .Qn(d_ff_5_qn), .preset(and_10_out), .reset(and_11_out));  // open: Q, en
  D_Flip_Flop d_ff_6 (
    .clk(nor_1_out), .D(d_ff_16_qn), .Qn(d_ff_6_qn), .preset(and_12_out), .reset(and_13_out));  // open: Q, en
  D_Flip_Flop d_ff_7 (
    .clk(nor_1_out), .D(d_ff_17_qn), .Qn(d_ff_7_qn), .preset(and_14_out), .reset(and_15_out));  // open: Q, en
  D_Flip_Flop d_ff_8 (
    .clk(nor_1_out), .D(d_ff_18_qn), .Qn(d_ff_8_qn), .preset(and_16_out), .reset(and_17_out));  // open: Q, en
  D_Flip_Flop d_ff_9 (
    .clk(nor_1_out), .D(d_ff_19_qn), .Qn(d_ff_9_qn), .preset(and_18_out), .reset(and_19_out));  // open: Q, en
  D_Flip_Flop d_ff_10 (
    .clk(nor_1_out), .D(d_ff_20_qn), .Qn(d_ff_10_qn), .preset(and_20_out), .reset(and_21_out));  // open: Q, en
  D_Flip_Flop d_ff_11 (
    .clk(nor_1_out), .D(d_ff_21_qn), .Qn(d_ff_11_qn), .preset(and_22_out), .reset(and_23_out));  // open: Q, en
  D_Flip_Flop d_ff_12 (.clk(nACLK), .D(d_ff_1_qn), .Qn(d_ff_12_qn));  // open: Q, preset, en, reset
  D_Flip_Flop d_ff_13 (.clk(nACLK), .D(d_ff_2_qn), .Qn(d_ff_13_qn));  // open: Q, preset, en, reset
  D_Flip_Flop d_ff_14 (.clk(nACLK), .D(d_ff_3_qn), .Qn(d_ff_14_qn));  // open: Q, preset, en, reset
  D_Flip_Flop d_ff_15 (.clk(nACLK), .D(d_ff_4_qn), .Qn(d_ff_15_qn));  // open: Q, preset, en, reset
  D_Flip_Flop d_ff_16 (.clk(nACLK), .D(d_ff_5_qn), .Qn(d_ff_16_qn));  // open: Q, preset, en, reset
  D_Flip_Flop d_ff_17 (.clk(nACLK), .D(d_ff_6_qn), .Qn(d_ff_17_qn));  // open: Q, preset, en, reset
  D_Flip_Flop d_ff_18 (.clk(nACLK), .D(d_ff_7_qn), .Qn(d_ff_18_qn));  // open: Q, preset, en, reset
  D_Flip_Flop d_ff_19 (.clk(nACLK), .D(d_ff_8_qn), .Qn(d_ff_19_qn));  // open: Q, preset, en, reset
  D_Flip_Flop d_ff_20 (.clk(nACLK), .D(d_ff_9_qn), .Qn(d_ff_20_qn));  // open: Q, preset, en, reset
  D_Flip_Flop d_ff_21 (.clk(nACLK), .D(d_ff_10_qn), .Qn(d_ff_21_qn));  // open: Q, preset, en, reset
  D_Flip_Flop d_ff_22 (.clk(nACLK), .D(d_ff_11_qn), .Qn(d_ff_22_qn));  // open: Q, preset, en, reset
  not not_13 (not_13_out, nor_5_out);
  not not_14 (not_14_out, d_ff_22_qn);
  nor nor_5 (nor_5_out, not_15_out, RES);
  nor nor_6 (nor_6_out, d_ff_12_qn, d_ff_13_qn, d_ff_14_qn, d_ff_15_qn, d_ff_16_qn, d_ff_17_qn, d_ff_18_qn, d_ff_19_qn, d_ff_20_qn, d_ff_21_qn, d_ff_22_qn);
  nor nor_7 (nor_7_out, d_ff_12_qn, d_ff_13_qn, d_ff_14_qn, d_ff_15_qn, d_ff_16_qn, d_ff_17_qn, d_ff_18_qn, d_ff_19_qn, d_ff_20_qn, d_ff_21_qn, not_14_out);
  not not_15 (not_15_out, nor_7_out);

  // Notes on the sheet:
  //   NOR1
  //   NOR2
  //   INV3
  //   NOR3
endmodule

module LFSR (
  input  RSTEP,
  input  ACLK,
  input  W400E,
  input  D7,
  input  NORND,
  output RNDOUT
);

  wire and_1_out, and_2_out, d_latch_1_q, dpos_1_q, dpos_2_q, dpos_3_q, dpos_4_q, dpos_5_q, dpos_6_q,
       dpos_7_q, dpos_8_q, dpos_9_q, dpos_10_q, dpos_11_q, dpos_12_q, dpos_13_q, dpos_14_q, dpos_15_q,
       multiplexer_1_out, nor_1_out, nor_2_out, nor_3_out, nor_4_out;

  and and_1 (and_1_out, ACLK, W400E);
  D_latch d_latch_1 (.En(and_1_out), .In(D7), .Q(d_latch_1_q));  // open: nQ
  nor nor_1 (nor_1_out, multiplexer_1_out, nor_4_out, dpos_15_q);
  and and_2 (and_2_out, multiplexer_1_out, dpos_15_q);
  nor nor_2 (nor_2_out, nor_1_out, and_2_out);
  Dpos dpos_1 (.Clk(RSTEP), .In(nor_2_out), .Q(dpos_1_q));  // open: nQ
  Dpos dpos_2 (.Clk(RSTEP), .In(dpos_1_q), .Q(dpos_2_q));  // open: nQ
  Dpos dpos_3 (.Clk(RSTEP), .In(dpos_2_q), .Q(dpos_3_q));  // open: nQ
  Dpos dpos_4 (.Clk(RSTEP), .In(dpos_3_q), .Q(dpos_4_q));  // open: nQ
  Dpos dpos_5 (.Clk(RSTEP), .In(dpos_4_q), .Q(dpos_5_q));  // open: nQ
  Dpos dpos_6 (.Clk(RSTEP), .In(dpos_5_q), .Q(dpos_6_q));  // open: nQ
  Dpos dpos_7 (.Clk(RSTEP), .In(dpos_6_q), .Q(dpos_7_q));  // open: nQ
  Dpos dpos_8 (.Clk(RSTEP), .In(dpos_7_q), .Q(dpos_8_q));  // open: nQ
  Dpos dpos_9 (.Clk(RSTEP), .In(dpos_8_q), .Q(dpos_9_q));  // open: nQ
  Dpos dpos_10 (.Clk(RSTEP), .In(dpos_9_q), .Q(dpos_10_q));  // open: nQ
  Dpos dpos_11 (.Clk(RSTEP), .In(dpos_10_q), .Q(dpos_11_q));  // open: nQ
  Dpos dpos_12 (.Clk(RSTEP), .In(dpos_11_q), .Q(dpos_12_q));  // open: nQ
  Dpos dpos_13 (.Clk(RSTEP), .In(dpos_12_q), .Q(dpos_13_q));  // open: nQ
  Dpos dpos_14 (.Clk(RSTEP), .In(dpos_13_q), .Q(dpos_14_q));  // open: nQ
  Dpos dpos_15 (.Clk(RSTEP), .In(dpos_14_q), .Q(dpos_15_q));  // open: nQ
  nor nor_3 (nor_3_out, dpos_15_q, NORND);
  Multiplexer multiplexer_1 (.in0(dpos_14_q), .in1(dpos_9_q), .out(multiplexer_1_out), .sel(d_latch_1_q));  // open: en
  not not_1 (RNDOUT, nor_3_out);
  nor nor_4 (nor_4_out, dpos_1_q, dpos_2_q, dpos_3_q, dpos_4_q, dpos_5_q, dpos_6_q, dpos_7_q, dpos_8_q, dpos_9_q, dpos_10_q, dpos_11_q, dpos_12_q, dpos_13_q, dpos_14_q, dpos_15_q);
endmodule

module Envelope_frequency_divider (
  input  nACLK,
  input  LOAD,
  input  STEP,
  input  RES,
  input  Vol0,
  input  Vol1,
  input  Vol2,
  input  Vol3,
  output Output
);

  wire and_1_out, and_2_out, and_3_out, and_4_out, and_5_out, and_6_out, and_7_out, and_8_out, d_ff_1_q,
       d_ff_1_qn, d_ff_2_q, d_ff_2_qn, d_ff_3_q, d_ff_3_qn, d_ff_4_q, d_ff_4_qn, d_ff_5_qn, d_ff_6_qn,
       d_ff_7_qn, d_ff_8_qn, multiplexer_1_out, multiplexer_2_out, multiplexer_3_out, multiplexer_4_out,
       nor_1_out, nor_2_out, nor_3_out, not_1_out, not_2_out, not_3_out, not_4_out, not_5_out, not_6_out,
       not_7_out, not_8_out, or_1_out, or_2_out, or_3_out, or_4_out;

  and and_1 (and_1_out, LOAD, Vol0);
  and and_2 (and_2_out, LOAD, not_1_out);
  not not_1 (not_1_out, Vol0);
  and and_3 (and_3_out, LOAD, Vol1);
  and and_4 (and_4_out, LOAD, not_2_out);
  not not_2 (not_2_out, Vol1);
  and and_5 (and_5_out, LOAD, Vol2);
  and and_6 (and_6_out, LOAD, not_3_out);
  not not_3 (not_3_out, Vol2);
  and and_7 (and_7_out, LOAD, Vol3);
  and and_8 (and_8_out, LOAD, not_4_out);
  not not_4 (not_4_out, Vol3);
  D_Flip_Flop d_ff_1 (
    .clk(STEP), .D(d_ff_5_qn), .Q(d_ff_1_q), .Qn(d_ff_1_qn), .preset(and_1_out), .reset(or_1_out));  // open: en
  or or_1 (or_1_out, RES, and_2_out);
  D_Flip_Flop d_ff_2 (
    .clk(STEP), .D(d_ff_6_qn), .Q(d_ff_2_q), .Qn(d_ff_2_qn), .preset(and_3_out), .reset(or_2_out));  // open: en
  or or_2 (or_2_out, RES, and_4_out);
  D_Flip_Flop d_ff_3 (
    .clk(STEP), .D(d_ff_7_qn), .Q(d_ff_3_q), .Qn(d_ff_3_qn), .preset(and_5_out), .reset(or_3_out));  // open: en
  or or_3 (or_3_out, RES, and_6_out);
  D_Flip_Flop d_ff_4 (
    .clk(STEP), .D(d_ff_8_qn), .Q(d_ff_4_q), .Qn(d_ff_4_qn), .preset(and_7_out), .reset(or_4_out));  // open: en
  or or_4 (or_4_out, RES, and_8_out);
  Multiplexer multiplexer_1 (.in0(d_ff_1_qn), .in1(d_ff_1_q), .out(multiplexer_1_out), .sel(1'b1));  // open: en
  not not_5 (not_5_out, 1'b1);
  Multiplexer multiplexer_2 (.in0(d_ff_2_qn), .in1(d_ff_2_q), .out(multiplexer_2_out), .sel(nor_1_out));  // open: en
  not not_6 (not_6_out, nor_1_out);
  Multiplexer multiplexer_3 (.in0(d_ff_3_qn), .in1(d_ff_3_q), .out(multiplexer_3_out), .sel(nor_2_out));  // open: en
  not not_7 (not_7_out, nor_2_out);
  Multiplexer multiplexer_4 (.in0(d_ff_4_qn), .in1(d_ff_4_q), .out(multiplexer_4_out), .sel(nor_3_out));  // open: en
  not not_8 (not_8_out, nor_3_out);
  D_Flip_Flop d_ff_5 (.clk(nACLK), .D(multiplexer_1_out), .Qn(d_ff_5_qn));  // open: Q, preset, en, reset
  D_Flip_Flop d_ff_6 (.clk(nACLK), .D(multiplexer_2_out), .Qn(d_ff_6_qn));  // open: Q, preset, en, reset
  D_Flip_Flop d_ff_7 (.clk(nACLK), .D(multiplexer_3_out), .Qn(d_ff_7_qn));  // open: Q, preset, en, reset
  D_Flip_Flop d_ff_8 (.clk(nACLK), .D(multiplexer_4_out), .Qn(d_ff_8_qn));  // open: Q, preset, en, reset
  nor nor_1 (nor_1_out, d_ff_1_q, not_5_out);
  nor nor_2 (nor_2_out, d_ff_2_q, not_6_out);
  nor nor_3 (nor_3_out, d_ff_3_q, not_7_out);
  nor nor_4 (Output, d_ff_4_q, not_8_out);
endmodule

module Envelope_Control (
  input  nACLK,
  input  nLFO1,
  input  W400F,
  input  Input_ERC,
  input  Input_OEC,
  input  RND_LC,
  output RELOAD,
  output LOAD,
  output STEP,
  output Estep,
  output Eres,
  output Output_OEC
);

  wire d_ff_1_q, d_ff_2_qn, d_ff_3_q, d_ff_4_q, d_ff_5_q, d_ff_6_q, nor_1_out, nor_3_out, nor_4_out,
       nor_7_out, not_1_out, not_2_out;

  nor nor_1 (nor_1_out, W400F, RELOAD);
  nor nor_2 (RELOAD, nor_1_out, nor_4_out);
  nor nor_3 (nor_3_out, RELOAD, Input_ERC);
  nor nor_4 (nor_4_out, nLFO1, d_ff_3_q);
  D_Flip_Flop d_ff_1 (.clk(nACLK), .D(nor_3_out), .Q(d_ff_1_q));  // open: Qn, preset, en, reset
  D_Flip_Flop d_ff_2 (.clk(nACLK), .D(nor_3_out), .Qn(d_ff_2_qn));  // open: Q, preset, en, reset
  D_Flip_Flop d_ff_3 (.clk(nACLK), .D(nor_1_out), .Q(d_ff_3_q));  // open: Qn, preset, en, reset
  D_Flip_Flop d_ff_4 (.clk(nACLK), .D(RELOAD), .Q(d_ff_4_q));  // open: Qn, preset, en, reset
  D_Flip_Flop d_ff_5 (.clk(nACLK), .D(Input_OEC), .Q(d_ff_5_q));  // open: Qn, preset, en, reset
  D_Flip_Flop d_ff_6 (.clk(nACLK), .D(Input_OEC), .Q(d_ff_6_q));  // open: Qn, preset, en, reset
  nor nor_5 (LOAD, nLFO1, d_ff_1_q);
  nor nor_6 (STEP, nLFO1, d_ff_2_qn);
  not not_1 (not_1_out, LOAD);
  nor nor_7 (nor_7_out, d_ff_4_q, d_ff_5_q);
  nand nand_1 (Output_OEC, d_ff_6_q, RND_LC);
  not not_2 (not_2_out, nor_7_out);
  nor nor_8 (Estep, not_1_out, not_2_out);
  nor nor_9 (Eres, not_1_out, nor_7_out);

  // Notes on the sheet:
  //   NORFF1
  //   NORFF2
  //   RELOAD
  //   NOR1
  //   NOR6
  //   NOR5
  //   NOR4
  //   INV1
  //   NOR2
  //   NAND
  //   NOR7
  //   INV2
  //   NOR8
endmodule

module Envelope_output_counter (
  input  nACLK,
  input  Input_OEC,
  input  Eres,
  input  Estep,
  input  RES,
  input  Reload,
  output Env0,
  output Env1,
  output Env2,
  output Env3,
  output Output_OEC
);

  wire and_1_out, and_2_out, and_3_out, and_4_out, and_5_out, and_6_out, and_7_out, and_8_out, d_ff_1_qn,
       d_ff_2_qn, d_ff_3_qn, d_ff_4_qn, d_ff_5_qn, d_ff_6_qn, d_ff_7_qn, d_ff_8_qn, multiplexer_1_out,
       multiplexer_2_out, multiplexer_3_out, multiplexer_4_out, nor_1_out, nor_2_out, nor_3_out, not_1_out,
       not_2_out, not_3_out, not_4_out, not_5_out, not_6_out, not_7_out, not_8_out, or_1_out, or_2_out,
       or_3_out, or_4_out;

  not not_1 (not_1_out, Input_OEC);
  not not_2 (not_2_out, Input_OEC);
  not not_3 (not_3_out, Input_OEC);
  not not_4 (not_4_out, Input_OEC);
  D_Flip_Flop d_ff_1 (
    .clk(Estep), .D(d_ff_5_qn), .Q(Env0), .Qn(d_ff_1_qn), .preset(and_1_out), .reset(or_1_out));  // open: en
  or or_1 (or_1_out, RES, and_2_out);
  and and_1 (and_1_out, Eres, Input_OEC);
  and and_2 (and_2_out, Eres, not_1_out);
  D_Flip_Flop d_ff_2 (
    .clk(Estep), .D(d_ff_6_qn), .Q(Env1), .Qn(d_ff_2_qn), .preset(and_3_out), .reset(or_2_out));  // open: en
  or or_2 (or_2_out, RES, and_4_out);
  and and_3 (and_3_out, Eres, Input_OEC);
  and and_4 (and_4_out, Eres, not_2_out);
  D_Flip_Flop d_ff_3 (
    .clk(Estep), .D(d_ff_7_qn), .Q(Env2), .Qn(d_ff_3_qn), .preset(and_5_out), .reset(or_3_out));  // open: en
  or or_3 (or_3_out, RES, and_6_out);
  and and_5 (and_5_out, Eres, Input_OEC);
  and and_6 (and_6_out, Eres, not_3_out);
  D_Flip_Flop d_ff_4 (
    .clk(Estep), .D(d_ff_8_qn), .Q(Env3), .Qn(d_ff_4_qn), .preset(and_7_out), .reset(or_4_out));  // open: en
  or or_4 (or_4_out, RES, and_8_out);
  and and_7 (and_7_out, Eres, Input_OEC);
  and and_8 (and_8_out, Eres, not_4_out);
  Multiplexer multiplexer_1 (.in0(d_ff_1_qn), .in1(Env0), .out(multiplexer_1_out), .sel(1'b1));  // open: en
  not not_5 (not_5_out, 1'b1);
  Multiplexer multiplexer_2 (.in0(d_ff_2_qn), .in1(Env1), .out(multiplexer_2_out), .sel(nor_1_out));  // open: en
  not not_6 (not_6_out, nor_1_out);
  Multiplexer multiplexer_3 (.in0(d_ff_3_qn), .in1(Env2), .out(multiplexer_3_out), .sel(nor_2_out));  // open: en
  not not_7 (not_7_out, nor_2_out);
  Multiplexer multiplexer_4 (.in0(d_ff_4_qn), .in1(Env3), .out(multiplexer_4_out), .sel(nor_3_out));  // open: en
  not not_8 (not_8_out, nor_3_out);
  D_Flip_Flop d_ff_5 (.clk(nACLK), .D(multiplexer_1_out), .Qn(d_ff_5_qn));  // open: Q, preset, en, reset
  D_Flip_Flop d_ff_6 (.clk(nACLK), .D(multiplexer_2_out), .Qn(d_ff_6_qn));  // open: Q, preset, en, reset
  D_Flip_Flop d_ff_7 (.clk(nACLK), .D(multiplexer_3_out), .Qn(d_ff_7_qn));  // open: Q, preset, en, reset
  D_Flip_Flop d_ff_8 (.clk(nACLK), .D(multiplexer_4_out), .Qn(d_ff_8_qn));  // open: Q, preset, en, reset
  nor nor_1 (nor_1_out, Env0, not_5_out);
  nor nor_2 (nor_2_out, Env1, not_6_out);
  nor nor_3 (nor_3_out, Env2, not_7_out);
  nor nor_4 (Output_OEC, Env3, Reload, not_8_out);
endmodule

module Masterclock (
  input  PHI0,
  input  RES,
  output PHI1,
  output PHI2,
  output ACLK,
  output nACLK
);

  wire d_ff_1_qn, d_ff_2_qn, nor_1_out, nor_2_out, not_2_out;

  not not_1 (PHI1, PHI0);
  not not_2 (not_2_out, PHI1);
  D_Flip_Flop d_ff_1 (.clk(PHI1), .D(nor_1_out), .Qn(d_ff_1_qn));  // open: Q, preset, en, reset
  D_Flip_Flop d_ff_2 (.clk(PHI0), .D(d_ff_1_qn), .Qn(d_ff_2_qn));  // open: Q, preset, en, reset
  nor nor_1 (nor_1_out, d_ff_2_qn, RES);
  nor nor_2 (nor_2_out, nor_1_out, not_2_out);
  nor nor_3 (nACLK, not_2_out, PHI0, d_ff_2_qn);
  not not_3 (ACLK, nor_2_out);

  assign PHI2 = PHI0;

  // Notes on the sheet:
  //   INV1
  //   DL1
  //   DL2
  //   NOR1
  //   NOR2
  //   NOR3
endmodule
