// Logisim project Primclockdivider.circ as structural Verilog: 1 circuit, main circuit main
module main (
  input  in_1,
  input  PHI2_CPU,
  output CLK,
  output nCLK,
  output PHI0_CPU,
  output M2_PIN
);

  wire clock_1_out, d_ff_1_qn, d_ff_2_qn, d_ff_3_qn, d_ff_4_qn, d_ff_5_qn, d_ff_6_qn, d_ff_7_qn, d_ff_8_qn,
       d_ff_9_q, d_ff_10_q, d_ff_11_q, d_ff_12_q, nor_3_out, nor_4_out, nor_5_out, nor_6_out, nor_7_out,
       nor_8_out, not_1_out, not_2_out;
  wire [15:0] counter_1_q;

  Clock clock_1 (.out(clock_1_out));
  not not_1 (not_1_out, clock_1_out);
  nor nor_1 (CLK, not_1_out, nCLK);
  not not_2 (not_2_out, not_1_out);
  D_Flip_Flop d_ff_1 (.clk(nCLK), .D(d_ff_8_qn), .Qn(d_ff_1_qn));  // open: Q, preset, en, reset
  D_Flip_Flop d_ff_2 (.clk(nCLK), .D(nor_3_out), .Qn(d_ff_2_qn));  // open: Q, preset, en, reset
  D_Flip_Flop d_ff_3 (.clk(nCLK), .D(nor_4_out), .Qn(d_ff_3_qn));  // open: Q, preset, en, reset
  D_Flip_Flop d_ff_4 (.clk(nCLK), .D(nor_5_out), .Qn(d_ff_4_qn));  // open: Q, preset, en, reset
  D_Flip_Flop d_ff_5 (.clk(nCLK), .D(nor_6_out), .Qn(d_ff_5_qn));  // open: Q, preset, en, reset
  D_Flip_Flop d_ff_6 (.clk(nCLK), .D(PHI0_CPU), .Qn(d_ff_6_qn));  // open: Q, preset, en, reset
  nor nor_2 (nCLK, CLK, not_2_out);
  D_Flip_Flop d_ff_7 (.clk(CLK), .D(d_ff_1_qn), .Qn(d_ff_7_qn));  // open: Q, preset, en, reset
  D_Flip_Flop d_ff_8 (.clk(CLK), .D(d_ff_2_qn), .Qn(d_ff_8_qn));  // open: Q, preset, en, reset
  D_Flip_Flop d_ff_9 (.clk(CLK), .D(d_ff_3_qn), .Q(d_ff_9_q));  // open: Qn, preset, en, reset
  D_Flip_Flop d_ff_10 (.clk(CLK), .D(d_ff_4_qn), .Q(d_ff_10_q));  // open: Qn, preset, en, reset
  D_Flip_Flop d_ff_11 (.clk(CLK), .D(d_ff_5_qn), .Q(d_ff_11_q));  // open: Qn, preset, en, reset
  D_Flip_Flop d_ff_12 (.clk(CLK), .D(d_ff_6_qn), .Q(d_ff_12_q));  // open: Qn, preset, en, reset
  Counter #(.width(16), .max('hffff)) counter_1 (
    .Q(counter_1_q), .clk(clock_1_out), .clr(in_1));  // open: load, D, count, carry
  not not_3 (PHI0_CPU, d_ff_7_qn);
  nor nor_3 (nor_3_out, nor_7_out, d_ff_9_q);
  nor nor_4 (nor_4_out, nor_7_out, d_ff_10_q);
  nor nor_5 (nor_5_out, nor_7_out, d_ff_11_q);
  nor nor_6 (nor_6_out, nor_7_out, d_ff_12_q);
  nor nor_7 (nor_7_out, d_ff_8_qn, PHI0_CPU);
  RAM #(.addrWidth(16), .dataWidth(1), .bus("asynch")) ram_1 (
    .addr(counter_1_q), .data(PHI0_CPU), .sel(1'b1), .ld(1'b0), .clr(in_1));
  nor nor_8 (nor_8_out, d_ff_2_qn, PHI2_CPU);
  not not_4 (M2_PIN, nor_8_out);

  // Notes on the sheet:
  //   INV1
  //   NOR1
  //   INV2
  //   NOR2
  //   M2 pin is invertor
endmodule
