// Logisim project SQAURE1mod.circ as structural Verilog: 2 circuits, main circuit SQAURE1
module SQAURE1 (
  input  W4000,
  input  W4001,
  input  W4002,
  input  W4003,
  input  D0,
  input  D1,
  input  D2,
  input  D3,
  input  D4,
  input  D5,
  input  D6,
  input  D7,
  output S0,
  output S1,
  output S2,
  output S3,
  output S4,
  output S5,
  output S6,
  output S7,
  output S8,
  output S9,
  output S10
);

  wire and_1_out, and_2_out, and_3_out, and_4_out, clock_1_out, d_latch_1_out_3, d_latch_1_out_4,
       d_latch_2_out_3, d_latch_2_out_4, d_latch_3_out_3, d_latch_3_out_4, d_latch_4_out_3, d_latch_4_out_4,
       d_latch_5_out_3, d_latch_5_out_4, d_latch_6_out_3, d_latch_6_out_4, d_latch_7_out_3, d_latch_7_out_4,
       d_latch_8_out_3, d_latch_8_out_4, d_latch_9_out_3, d_latch_9_out_4, d_latch_10_out_3,
       d_latch_10_out_4, d_latch_11_out_3, d_latch_11_out_4, d_latch_12_out_3, d_latch_13_out_3,
       d_latch_14_out_3, d_latch_15_out_3, multiplexer_1_out, multiplexer_2_out, multiplexer_3_out,
       multiplexer_4_out, multiplexer_5_out, multiplexer_6_out, multiplexer_7_out, multiplexer_8_out,
       multiplexer_9_out, multiplexer_10_out, multiplexer_11_out, multiplexer_12_out, multiplexer_13_out,
       multiplexer_14_out, multiplexer_15_out, multiplexer_16_out, multiplexer_17_out, multiplexer_18_out,
       multiplexer_19_out, multiplexer_20_out, multiplexer_21_out, multiplexer_22_out, multiplexer_23_out,
       multiplexer_24_out, multiplexer_25_out, multiplexer_26_out, multiplexer_27_out, multiplexer_28_out,
       multiplexer_29_out, multiplexer_30_out, multiplexer_31_out, multiplexer_32_out, multiplexer_33_out,
       multiplexer_34_out, multiplexer_35_out, multiplexer_36_out, multiplexer_37_out, multiplexer_38_out,
       multiplexer_39_out, multiplexer_40_out, multiplexer_41_out, multiplexer_42_out, multiplexer_43_out,
       multiplexer_44_out;

  Clock clock_1 (.out(clock_1_out));
  and and_1 (and_1_out, clock_1_out, W4002);
  and and_2 (and_2_out, clock_1_out, W4003);
  and and_3 (and_3_out, clock_1_out, W4001);
  and and_4 (and_4_out, clock_1_out, W4001);
  D_LATCH d_latch_1 (.in_1(and_1_out), .in_2(D0), .out_3(d_latch_1_out_3), .out_4(d_latch_1_out_4));
  D_LATCH d_latch_2 (.in_1(and_1_out), .in_2(D1), .out_3(d_latch_2_out_3), .out_4(d_latch_2_out_4));
  D_LATCH d_latch_3 (.in_1(and_1_out), .in_2(D2), .out_3(d_latch_3_out_3), .out_4(d_latch_3_out_4));
  D_LATCH d_latch_4 (.in_1(and_1_out), .in_2(D3), .out_3(d_latch_4_out_3), .out_4(d_latch_4_out_4));
  D_LATCH d_latch_5 (.in_1(and_1_out), .in_2(D4), .out_3(d_latch_5_out_3), .out_4(d_latch_5_out_4));
  D_LATCH d_latch_6 (.in_1(and_1_out), .in_2(D5), .out_3(d_latch_6_out_3), .out_4(d_latch_6_out_4));
  D_LATCH d_latch_7 (.in_1(and_1_out), .in_2(D6), .out_3(d_latch_7_out_3), .out_4(d_latch_7_out_4));
  D_LATCH d_latch_8 (.in_1(and_1_out), .in_2(D7), .out_3(d_latch_8_out_3), .out_4(d_latch_8_out_4));
  D_LATCH d_latch_9 (.in_1(and_2_out), .in_2(D0), .out_3(d_latch_9_out_3), .out_4(d_latch_9_out_4));
  D_LATCH d_latch_10 (.in_1(and_2_out), .in_2(D1), .out_3(d_latch_10_out_3), .out_4(d_latch_10_out_4));
  D_LATCH d_latch_11 (.in_1(and_2_out), .in_2(D2), .out_3(d_latch_11_out_3), .out_4(d_latch_11_out_4));
  D_LATCH d_latch_12 (.in_1(and_3_out), .in_2(D0), .out_3(d_latch_12_out_3));  // open: out_4
  D_LATCH d_latch_13 (.in_1(and_3_out), .in_2(D1), .out_3(d_latch_13_out_3));  // open: out_4
  D_LATCH d_latch_14 (.in_1(and_3_out), .in_2(D2), .out_3(d_latch_14_out_3));  // open: out_4
  D_LATCH d_latch_15 (.in_1(and_4_out), .in_2(D3), .out_3(d_latch_15_out_3));  // open: out_4
  Multiplexer multiplexer_1 (
    .in0(d_latch_1_out_4), .in1(d_latch_1_out_3), .out(multiplexer_1_out), .sel(d_latch_15_out_3));  // open: en
  Multiplexer multiplexer_2 (
    .in0(d_latch_2_out_4), .in1(d_latch_2_out_3), .out(multiplexer_2_out), .sel(d_latch_15_out_3));  // open: en
  Multiplexer multiplexer_3 (
    .in0(d_latch_3_out_4), .in1(d_latch_3_out_3), .out(multiplexer_3_out), .sel(d_latch_15_out_3));  // open: en
  Multiplexer multiplexer_4 (
    .in0(d_latch_4_out_4), .in1(d_latch_4_out_3), .out(multiplexer_4_out), .sel(d_latch_15_out_3));  // open: en
  Multiplexer multiplexer_5 (
    .in0(d_latch_5_out_4), .in1(d_latch_5_out_3), .out(multiplexer_5_out), .sel(d_latch_15_out_3));  // open: en
  Multiplexer multiplexer_6 (
    .in0(d_latch_6_out_4), .in1(d_latch_6_out_3), .out(multiplexer_6_out), .sel(d_latch_15_out_3));  // open: en
  Multiplexer multiplexer_7 (
    .in0(d_latch_7_out_4), .in1(d_latch_7_out_3), .out(multiplexer_7_out), .sel(d_latch_15_out_3));  // open: en
  Multiplexer multiplexer_8 (
    .in0(d_latch_8_out_4), .in1(d_latch_8_out_3), .out(multiplexer_8_out), .sel(d_latch_15_out_3));  // open: en
  Multiplexer multiplexer_9 (
    .in0(d_latch_9_out_4), .in1(d_latch_9_out_3), .out(multiplexer_9_out), .sel(d_latch_15_out_3));  // open: en
  Multiplexer multiplexer_10 (
    .in0(d_latch_10_out_4), .in1(d_latch_10_out_3), .out(multiplexer_10_out), .sel(d_latch_15_out_3));  // open: en
  Multiplexer multiplexer_11 (
    .in0(d_latch_11_out_4), .in1(d_latch_11_out_3), .out(multiplexer_11_out), .sel(d_latch_15_out_3));  // open: en
  Multiplexer multiplexer_12 (
    .in0(multiplexer_1_out), .in1(multiplexer_2_out), .out(multiplexer_12_out), .sel(d_latch_12_out_3));  // open: en
  Multiplexer multiplexer_13 (
    .in0(multiplexer_2_out), .in1(multiplexer_3_out), .out(multiplexer_13_out), .sel(d_latch_12_out_3));  // open: en
  Multiplexer multiplexer_14 (
    .in0(multiplexer_3_out), .in1(multiplexer_4_out), .out(multiplexer_14_out), .sel(d_latch_12_out_3));  // open: en
  Multiplexer multiplexer_15 (
    .in0(multiplexer_4_out), .in1(multiplexer_5_out), .out(multiplexer_15_out), .sel(d_latch_12_out_3));  // open: en
  Multiplexer multiplexer_16 (
    .in0(multiplexer_5_out), .in1(multiplexer_6_out), .out(multiplexer_16_out), .sel(d_latch_12_out_3));  // open: en
  Multiplexer multiplexer_17 (
    .in0(multiplexer_6_out), .in1(multiplexer_7_out), .out(multiplexer_17_out), .sel(d_latch_12_out_3));  // open: en
  Multiplexer multiplexer_18 (
    .in0(multiplexer_7_out), .in1(multiplexer_8_out), .out(multiplexer_18_out), .sel(d_latch_12_out_3));  // open: en
  Multiplexer multiplexer_19 (
    .in0(multiplexer_8_out), .in1(multiplexer_9_out), .out(multiplexer_19_out), .sel(d_latch_12_out_3));  // open: en
  Multiplexer multiplexer_20 (
    .in0(multiplexer_9_out), .in1(multiplexer_10_out), .out(multiplexer_20_out), .sel(d_latch_12_out_3));  // open: en
  Multiplexer multiplexer_21 (
    .in0(multiplexer_10_out), .in1(multiplexer_11_out), .out(multiplexer_21_out), .sel(d_latch_12_out_3));  // open: en
  Multiplexer multiplexer_22 (
    .in0(multiplexer_11_out), .in1(d_latch_15_out_3), .out(multiplexer_22_out), .sel(d_latch_12_out_3));  // open: en
  Multiplexer multiplexer_23 (
    .in0(multiplexer_12_out), .in1(multiplexer_14_out), .out(multiplexer_23_out), .sel(d_latch_13_out_3));  // open: en
  Multiplexer multiplexer_24 (
    .in0(multiplexer_13_out), .in1(multiplexer_15_out), .out(multiplexer_24_out), .sel(d_latch_13_out_3));  // open: en
  Multiplexer multiplexer_25 (
    .in0(multiplexer_14_out), .in1(multiplexer_16_out), .out(multiplexer_25_out), .sel(d_latch_13_out_3));  // open: en
  Multiplexer multiplexer_26 (
    .in0(multiplexer_15_out), .in1(multiplexer_17_out), .out(multiplexer_26_out), .sel(d_latch_13_out_3));  // open: en
  Multiplexer multiplexer_27 (
    .in0(multiplexer_16_out), .in1(multiplexer_18_out), .out(multiplexer_27_out), .sel(d_latch_13_out_3));  // open: en
  Multiplexer multiplexer_28 (
    .in0(multiplexer_17_out), .in1(multiplexer_19_out), .out(multiplexer_28_out), .sel(d_latch_13_out_3));  // open: en
  Multiplexer multiplexer_29 (
    .in0(multiplexer_18_out), .in1(multiplexer_20_out), .out(multiplexer_29_out), .sel(d_latch_13_out_3));  // open: en
  Multiplexer multiplexer_30 (
    .in0(multiplexer_19_out), .in1(multiplexer_21_out), .out(multiplexer_30_out), .sel(d_latch_13_out_3));  // open: en
  Multiplexer multiplexer_31 (
    .in0(multiplexer_20_out), .in1(multiplexer_22_out), .out(multiplexer_31_out), .sel(d_latch_13_out_3));  // open: en
  Multiplexer multiplexer_32 (
    .in0(multiplexer_21_out), .in1(d_latch_15_out_3), .out(multiplexer_32_out), .sel(d_latch_13_out_3));  // open: en
  Multiplexer multiplexer_33 (
    .in0(multiplexer_22_out), .in1(d_latch_15_out_3), .out(multiplexer_33_out), .sel(d_latch_13_out_3));  // open: en
  Multiplexer multiplexer_34 (
    .in0(multiplexer_23_out), .in1(multiplexer_27_out), .out(multiplexer_34_out), .sel(d_latch_14_out_3));  // open: en
  Multiplexer multiplexer_35 (
    .in0(multiplexer_24_out), .in1(multiplexer_28_out), .out(multiplexer_35_out), .sel(d_latch_14_out_3));  // open: en
  Multiplexer multiplexer_36 (
    .in0(multiplexer_25_out), .in1(multiplexer_29_out), .out(multiplexer_36_out), .sel(d_latch_14_out_3));  // open: en
  Multiplexer multiplexer_37 (
    .in0(multiplexer_26_out), .in1(multiplexer_30_out), .out(multiplexer_37_out), .sel(d_latch_14_out_3));  // open: en
  Multiplexer multiplexer_38 (
    .in0(multiplexer_27_out), .in1(multiplexer_31_out), .out(multiplexer_38_out), .sel(d_latch_14_out_3));  // open: en
  Multiplexer multiplexer_39 (
    .in0(multiplexer_28_out), .in1(multiplexer_32_out), .out(multiplexer_39_out), .sel(d_latch_14_out_3));  // open: en
  Multiplexer multiplexer_40 (
    .in0(multiplexer_29_out), .in1(multiplexer_33_out), .out(multiplexer_40_out), .sel(d_latch_14_out_3));  // open: en
  Multiplexer multiplexer_41 (
    .in0(multiplexer_30_out), .in1(d_latch_15_out_3), .out(multiplexer_41_out), .sel(d_latch_14_out_3));  // open: en
  Multiplexer multiplexer_42 (
    .in0(multiplexer_31_out), .in1(d_latch_15_out_3), .out(multiplexer_42_out), .sel(d_latch_14_out_3));  // open: en
  Multiplexer multiplexer_43 (
    .in0(multiplexer_32_out), .in1(d_latch_15_out_3), .out(multiplexer_43_out), .sel(d_latch_14_out_3));  // open: en
  Multiplexer multiplexer_44 (
    .in0(multiplexer_33_out), .in1(d_latch_15_out_3), .out(multiplexer_44_out), .sel(d_latch_14_out_3));  // open: en
  not not_1 (S0, multiplexer_34_out);
  not not_2 (S1, multiplexer_35_out);
  not not_3 (S2, multiplexer_36_out);
  not not_4 (S3, multiplexer_37_out);
  not not_5 (S4, multiplexer_38_out);
  not not_6 (S5, multiplexer_39_out);
  not not_7 (S6, multiplexer_40_out);
  not not_8 (S7, multiplexer_41_out);
  not not_9 (S8, multiplexer_42_out);
  not not_10 (S9, multiplexer_43_out);
  not not_11 (S10, multiplexer_44_out);

  // Notes on the sheet:
  //   FREQ IN
  //   SHIFT IN
  //   SHIFT DIRECTION
  //   DEC
  //   BARREL SHIFTER
endmodule

module D_LATCH (
  input  in_1,
  input  in_2,
  output out_3,
  output out_4
);

  D_Flip_Flop #(.trigger("high")) d_ff_1 (.clk(in_1), .D(in_2), .Q(out_3), .Qn(out_4));  // open: preset, en, reset
endmodule
