// Logisim project Squarechannelrev.circ as structural Verilog: 9 circuits, main circuit main
module main (
  input  in_1,
  input  W4000,
  input  in_3,
  input  W4001,
  input  W4002,
  input  W4003,
  input  D0,
  input  D1,
  input  D2,
  input  D3,
  input  D4,
  input  D5,
  input  D6,
  input  D7,
  input  nLFO2,
  input  nLFO1,
  input  NOSQA,
  input  RES,
  output SQA0,
  output SQA1,
  output SQ2,
  output SQA3
);

  wire adder_1_ncout, adder_1_sweep, clock_1_out, d_ff_1_qn, divider_1_sqout, envelope_generator_1_env0,
       envelope_generator_1_env1, envelope_generator_1_env2, envelope_generator_1_env3,
       envelope_generator_1_envdis, envelope_generator_1_vol0, envelope_generator_1_vol1,
       envelope_generator_1_vol2, envelope_generator_1_vol3, masterclock_1_aclk, masterclock_1_naclk,
       masterclock_1_phi2, multiplexer_1_out, multiplexer_2_out, multiplexer_3_out, multiplexer_4_out,
       nor_1_out, not_1_out, not_2_out, not_3_out, not_4_out, not_5_out, sweepcontrol_1_addout,
       sweepcontrol_1_d_i, sweepcontrol_1_sr0, sweepcontrol_1_sr1, sweepcontrol_1_sr2, sweepcontrol_1_swctrl,
       sweepcontrol_1_sweep_2;
  wire [10:0] adder_1_pl0, register_1_q;
  wire [15:0] counter_1_q, register_2_q;

  Clock clock_1 (.out(clock_1_out));
  Masterclock masterclock_1 (
    .PHI0(clock_1_out), .RES(RES), .PHI2(masterclock_1_phi2), .ACLK(masterclock_1_aclk),
    .nACLK(masterclock_1_naclk));  // open: PHI1
  // Probe on register_1_q
  // Probe on adder_1_pl0
  Register #(.width(11)) register_1 (.D(adder_1_pl0), .Q(register_1_q), .clk(in_1), .clr(in_3));  // open: en
  Adder adder_1 (
    .nACLK(masterclock_1_naclk), .ACLK(masterclock_1_aclk), .W4002(W4002), .W4003(W4003), .D0(D0), .D1(D1),
    .D2(D2), .D3(D3), .D4(D4), .D5(D5), .D6(D6), .D7(D7), .Dec_Inc(sweepcontrol_1_d_i),
    .SR0(sweepcontrol_1_sr0), .SR1(sweepcontrol_1_sr1), .SR2(sweepcontrol_1_sr2),
    .Addout(sweepcontrol_1_addout), .PL0(adder_1_pl0[0]), .PL1(adder_1_pl0[1]), .PL2(adder_1_pl0[2]),
    .PL3(adder_1_pl0[3]), .PL4(adder_1_pl0[4]), .PL5(adder_1_pl0[5]), .PL6(adder_1_pl0[6]),
    .PL7(adder_1_pl0[7]), .PL8(adder_1_pl0[8]), .PL9(adder_1_pl0[9]), .PL10(adder_1_pl0[10]),
    .nCOUT(adder_1_ncout), .SWEEP(adder_1_sweep));
  SweepControl sweepcontrol_1 (
    .nACLK(masterclock_1_naclk), .ACLK(masterclock_1_aclk), .W4001(W4001), .D0(D0), .D1(D1), .D2(D2),
    .D3(D3), .D4(D4), .D5(D5), .D6(D6), .D7(D7), .nLFO2(nLFO2), .NOSQA(NOSQA), .nCOUT(adder_1_ncout),
    .SWEEP(adder_1_sweep), .RES(RES), .SR0(sweepcontrol_1_sr0), .SR1(sweepcontrol_1_sr1),
    .SR2(sweepcontrol_1_sr2), .D_I(sweepcontrol_1_d_i), .ADDOUT(sweepcontrol_1_addout),
    .SWEEP_2(sweepcontrol_1_sweep_2), .SWCTRL(sweepcontrol_1_swctrl));
  not not_1 (not_1_out, divider_1_sqout);
  Divider divider_1 (
    .ACLK(masterclock_1_aclk), .W4000(W4000), .W4003(W4003), .RES(RES), .PL0(adder_1_pl0[0]),
    .PL1(adder_1_pl0[1]), .PL2(adder_1_pl0[2]), .PL3(adder_1_pl0[3]), .PL4(adder_1_pl0[4]),
    .PL5(adder_1_pl0[5]), .PL6(adder_1_pl0[6]), .PL7(adder_1_pl0[7]), .PL8(adder_1_pl0[8]),
    .PL9(adder_1_pl0[9]), .PL10(adder_1_pl0[10]), .D6(D6), .D7(D7), .SQOUT(divider_1_sqout),
    .nACLK(masterclock_1_naclk));  // open: FLOAD
  nor nor_1 (nor_1_out, not_1_out, sweepcontrol_1_sweep_2, sweepcontrol_1_swctrl, NOSQA);
  Counter #(.width(16), .max('hffff)) counter_1 (
    .Q(counter_1_q), .clk(masterclock_1_phi2), .clr(divider_1_sqout));  // open: load, D, count, carry
  D_Flip_Flop d_ff_1 (.clk(masterclock_1_naclk), .D(nor_1_out), .Qn(d_ff_1_qn));  // open: Q, preset, en, reset
  Register #(.width(16)) register_2 (.D(counter_1_q), .Q(register_2_q), .clk(divider_1_sqout));  // open: en, clr
  // Probe on register_2_q
  nor nor_2 (SQA0, not_2_out, d_ff_1_qn);
  nor nor_3 (SQA1, not_3_out, d_ff_1_qn);
  nor nor_4 (SQ2, not_4_out, d_ff_1_qn);
  nor nor_5 (SQA3, not_5_out, d_ff_1_qn);
  Envelope_Generator envelope_generator_1 (
    .nACLK(masterclock_1_naclk), .ACLK(masterclock_1_aclk), .W4000(W4000), .W4003(W4003), .D0(D0), .D1(D1),
    .D2(D2), .D3(D3), .D4(D4), .D5(D5), .nLFO1(nLFO1), .RES(RES), .VOL0(envelope_generator_1_vol0),
    .VOL1(envelope_generator_1_vol1), .VOL2(envelope_generator_1_vol2), .ENVDIS(envelope_generator_1_envdis),
    .VOL3(envelope_generator_1_vol3), .Env0(envelope_generator_1_env0), .Env1(envelope_generator_1_env1),
    .Env2(envelope_generator_1_env2), .Env3(envelope_generator_1_env3));
  not not_2 (not_2_out, multiplexer_1_out);
  Multiplexer multiplexer_1 (
    .in0(envelope_generator_1_env0), .in1(envelope_generator_1_vol0), .out(multiplexer_1_out),
    .sel(envelope_generator_1_envdis));  // open: en
  not not_3 (not_3_out, multiplexer_2_out);
  Multiplexer multiplexer_2 (
    .in0(envelope_generator_1_env1), .in1(envelope_generator_1_vol1), .out(multiplexer_2_out),
    .sel(envelope_generator_1_envdis));  // open: en
  not not_4 (not_4_out, multiplexer_3_out);
  Multiplexer multiplexer_3 (
    .in0(envelope_generator_1_env2), .in1(envelope_generator_1_vol2), .out(multiplexer_3_out),
    .sel(envelope_generator_1_envdis));  // open: en
  not not_5 (not_5_out, multiplexer_4_out);
  Multiplexer multiplexer_4 (
    .in0(envelope_generator_1_env3), .in1(envelope_generator_1_vol3), .out(multiplexer_4_out),
    .sel(envelope_generator_1_envdis));  // open: en

  // Notes on the sheet:
  //   INV5
  //   DL5
endmodule

module Adder (
  input  nACLK,
  input  ACLK,
  input  W4002,
  input  W4003,
  input  D0,
  input  D1,
  input  D2,
  input  D3,
  input  D4,
  input  D5,
  input  D6,
  input  D7,
  input  Dec_Inc,
  input  SR0,
  input  SR1,
  input  SR2,
  input  Addout,
  output PL0,
  output PL1,
  output PL2,
  output PL3,
  output PL4,
  output PL5,
  output PL6,
  output PL7,
  output PL8,
  output PL9,
  output PL10,
  output nCOUT,
  output SWEEP
);

  wire addercell_1_ncarryout, addercell_1_nsum, addercell_2_ncarryout, addercell_2_nsum,
       addercell_3_ncarryout, addercell_3_nsum, addercell_4_ncarryout, addercell_4_nsum,
       addercell_5_ncarryout, addercell_5_nsum, addercell_6_ncarryout, addercell_6_nsum,
       addercell_7_ncarryout, addercell_7_nsum, addercell_8_ncarryout, addercell_8_nsum,
       addercell_9_ncarryout, addercell_9_nsum, addercell_10_ncarryout, addercell_10_nsum, addercell_11_nsum,
       barrelshifter_1_s0, barrelshifter_1_s1, barrelshifter_1_s2, barrelshifter_1_s3, barrelshifter_1_s4,
       barrelshifter_1_s5, barrelshifter_1_s6, barrelshifter_1_s7, barrelshifter_1_s8, barrelshifter_1_s9,
       barrelshifter_1_s10, not_1_out, register_1_f0, register_1_f1, register_1_f2, register_1_f3,
       register_1_f4, register_1_f5, register_1_f6, register_1_f7, register_1_f8, register_1_f9,
       register_1_f10, register_1_mu0, register_1_mu1, register_1_mu2, register_1_mu3, register_1_mu4,
       register_1_mu5, register_1_mu6, register_1_mu7, register_1_mu8, register_1_mu9, register_1_mu10,
       register_1_nf0, register_1_nf1, register_1_nf2, register_1_nf3, register_1_nf4, register_1_nf5,
       register_1_nf6, register_1_nf7, register_1_nf8, register_1_nf9, register_1_nf10;

  register register_1 (
    .nACLK(nACLK), .ACLK(ACLK), .W4002(W4002), .W4003(W4003), .D0(D0), .D1(D1), .D2(D2), .D3(D3), .D4(D4),
    .D5(D5), .D6(D6), .D7(D7), .D_I(Dec_Inc), .F0(register_1_f0), .nF0(register_1_nf0), .MU0(register_1_mu0),
    .nSum0(addercell_1_nsum), .F1(register_1_f1), .nF1(register_1_nf1), .MU1(register_1_mu1),
    .nSum1(addercell_2_nsum), .F2(register_1_f2), .nF2(register_1_nf2), .MU2(register_1_mu2),
    .nSum2(addercell_3_nsum), .F3(register_1_f3), .nF3(register_1_nf3), .MU3(register_1_mu3),
    .nSum3(addercell_4_nsum), .F4(register_1_f4), .nF4(register_1_nf4), .MU4(register_1_mu4),
    .nSum4(addercell_5_nsum), .F5(register_1_f5), .nF5(register_1_nf5), .MU5(register_1_mu5),
    .nSum5(addercell_6_nsum), .F6(register_1_f6), .nF6(register_1_nf6), .MU6(register_1_mu6),
    .nSum6(addercell_7_nsum), .F7(register_1_f7), .nF7(register_1_nf7), .MU7(register_1_mu7),
    .nSum7(addercell_8_nsum), .F8(register_1_f8), .nF8(register_1_nf8), .MU8(register_1_mu8),
    .nSum8(addercell_9_nsum), .F9(register_1_f9), .nF9(register_1_nf9), .MU9(register_1_mu9),
    .nSum9(addercell_10_nsum), .F10(register_1_f10), .nF10(register_1_nf10), .MU10(register_1_mu10),
    .Addout(Addout), .nSum10(addercell_11_nsum));
  Barrelshifter barrelshifter_1 (
    .MUI0(register_1_mu0), .MUI1(register_1_mu1), .MUI2(register_1_mu2), .MUI3(register_1_mu3),
    .MUI4(register_1_mu4), .MUI5(register_1_mu5), .MUI6(register_1_mu6), .MUI7(register_1_mu7),
    .MUI8(register_1_mu8), .MUI9(register_1_mu9), .MUI10(register_1_mu10), .Dec_Inc(Dec_Inc), .SR0(SR0),
    .SR1(SR1), .SR2(SR2), .S0(barrelshifter_1_s0), .S1(barrelshifter_1_s1), .S2(barrelshifter_1_s2),
    .S3(barrelshifter_1_s3), .S4(barrelshifter_1_s4), .S5(barrelshifter_1_s5), .S6(barrelshifter_1_s6),
    .S7(barrelshifter_1_s7), .S8(barrelshifter_1_s8), .S9(barrelshifter_1_s9), .S10(barrelshifter_1_s10));
  not not_1 (not_1_out, Dec_Inc);
  Addercell addercell_1 (
    .nCX(1'b1), .FX(register_1_f0), .nFX(register_1_nf0), .SX(barrelshifter_1_s0), .FX_2(PL0),
    .nSum(addercell_1_nsum), .nCarryOut(addercell_1_ncarryout));
  Addercell addercell_2 (
    .nCX(addercell_1_ncarryout), .FX(register_1_f1), .nFX(register_1_nf1), .SX(barrelshifter_1_s1),
    .FX_2(PL1), .nSum(addercell_2_nsum), .nCarryOut(addercell_2_ncarryout));
  Addercell addercell_3 (
    .nCX(addercell_2_ncarryout), .FX(register_1_f2), .nFX(register_1_nf2), .SX(barrelshifter_1_s2),
    .FX_2(PL2), .nSum(addercell_3_nsum), .nCarryOut(addercell_3_ncarryout));
  Addercell addercell_4 (
    .nCX(addercell_3_ncarryout), .FX(register_1_f3), .nFX(register_1_nf3), .SX(barrelshifter_1_s3),
    .FX_2(PL3), .nSum(addercell_4_nsum), .nCarryOut(addercell_4_ncarryout));
  Addercell addercell_5 (
    .nCX(addercell_4_ncarryout), .FX(register_1_f4), .nFX(register_1_nf4), .SX(barrelshifter_1_s4),
    .FX_2(PL4), .nSum(addercell_5_nsum), .nCarryOut(addercell_5_ncarryout));
  Addercell addercell_6 (
    .nCX(addercell_5_ncarryout), .FX(register_1_f5), .nFX(register_1_nf5), .SX(barrelshifter_1_s5),
    .FX_2(PL5), .nSum(addercell_6_nsum), .nCarryOut(addercell_6_ncarryout));
  Addercell addercell_7 (
    .nCX(addercell_6_ncarryout), .FX(register_1_f6), .nFX(register_1_nf6), .SX(barrelshifter_1_s6),
    .FX_2(PL6), .nSum(addercell_7_nsum), .nCarryOut(addercell_7_ncarryout));
  Addercell addercell_8 (
    .nCX(addercell_7_ncarryout), .FX(register_1_f7), .nFX(register_1_nf7), .SX(barrelshifter_1_s7),
    .FX_2(PL7), .nSum(addercell_8_nsum), .nCarryOut(addercell_8_ncarryout));
  Addercell addercell_9 (
    .nCX(addercell_8_ncarryout), .FX(register_1_f8), .nFX(register_1_nf8), .SX(barrelshifter_1_s8),
    .FX_2(PL8), .nSum(addercell_9_nsum), .nCarryOut(addercell_9_ncarryout));
  Addercell addercell_10 (
    .nCX(addercell_9_ncarryout), .FX(register_1_f9), .nFX(register_1_nf9), .SX(barrelshifter_1_s9),
    .FX_2(PL9), .nSum(addercell_10_nsum), .nCarryOut(addercell_10_ncarryout));
  Addercell addercell_11 (
    .nCX(addercell_10_ncarryout), .FX(register_1_f10), .nFX(register_1_nf10), .SX(barrelshifter_1_s10),
    .FX_2(PL10), .nSum(addercell_11_nsum), .nCarryOut(nCOUT));
  nor nor_1 (SWEEP, PL2, PL3, PL4, PL5, PL6, PL7, PL8, PL9, PL10);

  // Notes on the sheet:
  //   INC
  //   Connect to VCC for square1, connect to inverter for square2
endmodule

module register (
  input  nACLK,
  input  ACLK,
  input  W4002,
  input  W4003,
  input  D0,
  input  nSum0,
  input  D1,
  input  nSum1,
  input  D2,
  input  nSum2,
  input  D3,
  input  nSum3,
  input  D4,
  input  nSum4,
  input  D5,
  input  nSum5,
  input  D6,
  input  nSum6,
  input  D7,
  input  nSum7,
  input  nSum8,
  input  nSum9,
  input  Addout,
  input  nSum10,
  input  D_I,
  output F0,
  output nF0,
  output MU0,
  output F1,
  output nF1,
  output MU1,
  output F2,
  output nF2,
  output MU2,
  output F3,
  output nF3,
  output MU3,
  output F4,
  output nF4,
  output MU4,
  output F5,
  output nF5,
  output MU5,
  output F6,
  output nF6,
  output MU6,
  output F7,
  output nF7,
  output MU7,
  output F8,
  output nF8,
  output MU8,
  output F9,
  output nF9,
  output MU9,
  output F10,
  output nF10,
  output MU10
);

  wire and_1_out, and_2_out, and_3_out, and_4_out, and_5_out, and_6_out, and_7_out, and_8_out, and_9_out,
       and_10_out, and_11_out, and_12_out, and_13_out, and_14_out, and_15_out, and_16_out, and_17_out,
       and_18_out, and_19_out, and_20_out, and_21_out, and_22_out, and_23_out, and_24_out, and_25_out,
       and_26_out, and_27_out, and_28_out, and_29_out, and_30_out, and_31_out, and_32_out, and_33_out,
       d_ff_1_q, d_ff_1_qn, d_ff_2_q, d_ff_2_qn, d_ff_3_q, d_ff_3_qn, d_ff_4_q, d_ff_4_qn, d_ff_5_q,
       d_ff_5_qn, d_ff_6_q, d_ff_6_qn, d_ff_7_q, d_ff_7_qn, d_ff_8_q, d_ff_8_qn, d_ff_9_q, d_ff_9_qn,
       d_ff_10_q, d_ff_10_qn, d_ff_11_q, d_ff_11_qn;

  and and_1 (and_1_out, ACLK, W4002);
  and and_2 (and_2_out, Addout, d_ff_1_q);
  D_Flip_Flop d_ff_1 (.clk(nACLK), .D(nSum0), .Q(d_ff_1_q), .Qn(d_ff_1_qn));  // open: preset, en, reset
  and and_3 (and_3_out, Addout, d_ff_1_qn);
  and and_4 (and_4_out, ACLK, W4002);
  and and_5 (and_5_out, Addout, d_ff_2_q);
  D_Flip_Flop d_ff_2 (.clk(nACLK), .D(nSum1), .Q(d_ff_2_q), .Qn(d_ff_2_qn));  // open: preset, en, reset
  and and_6 (and_6_out, Addout, d_ff_2_qn);
  and and_7 (and_7_out, ACLK, W4002);
  and and_8 (and_8_out, Addout, d_ff_3_q);
  D_Flip_Flop d_ff_3 (.clk(nACLK), .D(nSum2), .Q(d_ff_3_q), .Qn(d_ff_3_qn));  // open: preset, en, reset
  and and_9 (and_9_out, Addout, d_ff_3_qn);
  and and_10 (and_10_out, ACLK, W4002);
  and and_11 (and_11_out, Addout, d_ff_4_q);
  D_Flip_Flop d_ff_4 (.clk(nACLK), .D(nSum3), .Q(d_ff_4_q), .Qn(d_ff_4_qn));  // open: preset, en, reset
  and and_12 (and_12_out, Addout, d_ff_4_qn);
  and and_13 (and_13_out, ACLK, W4002);
  and and_14 (and_14_out, Addout, d_ff_5_q);
  D_Flip_Flop d_ff_5 (.clk(nACLK), .D(nSum4), .Q(d_ff_5_q), .Qn(d_ff_5_qn));  // open: preset, en, reset
  and and_15 (and_15_out, Addout, d_ff_5_qn);
  and and_16 (and_16_out, ACLK, W4002);
  and and_17 (and_17_out, Addout, d_ff_6_q);
  D_Flip_Flop d_ff_6 (.clk(nACLK), .D(nSum5), .Q(d_ff_6_q), .Qn(d_ff_6_qn));  // open: preset, en, reset
  and and_18 (and_18_out, Addout, d_ff_6_qn);
  and and_19 (and_19_out, ACLK, W4002);
  and and_20 (and_20_out, Addout, d_ff_7_q);
  D_Flip_Flop d_ff_7 (.clk(nACLK), .D(nSum6), .Q(d_ff_7_q), .Qn(d_ff_7_qn));  // open: preset, en, reset
  and and_21 (and_21_out, Addout, d_ff_7_qn);
  and and_22 (and_22_out, ACLK, W4002);
  and and_23 (and_23_out, Addout, d_ff_8_q);
  D_Flip_Flop d_ff_8 (.clk(nACLK), .D(nSum7), .Q(d_ff_8_q), .Qn(d_ff_8_qn));  // open: preset, en, reset
  and and_24 (and_24_out, Addout, d_ff_8_qn);
  and and_25 (and_25_out, ACLK, W4003);
  and and_26 (and_26_out, Addout, d_ff_9_q);
  D_Flip_Flop d_ff_9 (.clk(nACLK), .D(nSum8), .Q(d_ff_9_q), .Qn(d_ff_9_qn));  // open: preset, en, reset
  and and_27 (and_27_out, Addout, d_ff_9_qn);
  and and_28 (and_28_out, ACLK, W4003);
  and and_29 (and_29_out, Addout, d_ff_10_q);
  D_Flip_Flop d_ff_10 (.clk(nACLK), .D(nSum9), .Q(d_ff_10_q), .Qn(d_ff_10_qn));  // open: preset, en, reset
  and and_30 (and_30_out, Addout, d_ff_10_qn);
  and and_31 (and_31_out, ACLK, W4003);
  and and_32 (and_32_out, Addout, d_ff_11_q);
  D_Flip_Flop d_ff_11 (.clk(nACLK), .D(nSum10), .Q(d_ff_11_q), .Qn(d_ff_11_qn));  // open: preset, en, reset
  and and_33 (and_33_out, Addout, d_ff_11_qn);
  D_Flip_Flop d_ff_12 (.clk(and_1_out), .D(D0), .Q(F0), .Qn(nF0), .preset(and_3_out), .reset(and_2_out));  // open: en
  D_Flip_Flop d_ff_13 (.clk(and_4_out), .D(D1), .Q(F1), .Qn(nF1), .preset(and_6_out), .reset(and_5_out));  // open: en
  D_Flip_Flop d_ff_14 (.clk(and_7_out), .D(D2), .Q(F2), .Qn(nF2), .preset(and_9_out), .reset(and_8_out));  // open: en
  D_Flip_Flop d_ff_15 (
    .clk(and_10_out), .D(D3), .Q(F3), .Qn(nF3), .preset(and_12_out), .reset(and_11_out));  // open: en
  D_Flip_Flop d_ff_16 (
    .clk(and_13_out), .D(D4), .Q(F4), .Qn(nF4), .preset(and_15_out), .reset(and_14_out));  // open: en
  D_Flip_Flop d_ff_17 (
    .clk(and_16_out), .D(D5), .Q(F5), .Qn(nF5), .preset(and_18_out), .reset(and_17_out));  // open: en
  D_Flip_Flop d_ff_18 (
    .clk(and_19_out), .D(D6), .Q(F6), .Qn(nF6), .preset(and_21_out), .reset(and_20_out));  // open: en
  D_Flip_Flop d_ff_19 (
    .clk(and_22_out), .D(D7), .Q(F7), .Qn(nF7), .preset(and_24_out), .reset(and_23_out));  // open: en
  D_Flip_Flop d_ff_20 (
    .clk(and_25_out), .D(D0), .Q(F8), .Qn(nF8), .preset(and_27_out), .reset(and_26_out));  // open: en
  D_Flip_Flop d_ff_21 (
    .clk(and_28_out), .D(D1), .Q(F9), .Qn(nF9), .preset(and_30_out), .reset(and_29_out));  // open: en
  D_Flip_Flop d_ff_22 (
    .clk(and_31_out), .D(D2), .Q(F10), .Qn(nF10), .preset(and_33_out), .reset(and_32_out));  // open: en
  Multiplexer multiplexer_1 (.in0(F0), .in1(nF0), .out(MU0), .sel(D_I));  // open: en
  Multiplexer multiplexer_2 (.in0(F1), .in1(nF1), .out(MU1), .sel(D_I));  // open: en
  Multiplexer multiplexer_3 (.in0(F2), .in1(nF2), .out(MU2), .sel(D_I));  // open: en
  Multiplexer multiplexer_4 (.in0(F3), .in1(nF3), .out(MU3), .sel(D_I));  // open: en
  Multiplexer multiplexer_5 (.in0(F4), .in1(nF4), .out(MU4), .sel(D_I));  // open: en
  Multiplexer multiplexer_6 (.in0(F5), .in1(nF5), .out(MU5), .sel(D_I));  // open: en
  Multiplexer multiplexer_7 (.in0(F6), .in1(nF6), .out(MU6), .sel(D_I));  // open: en
  Multiplexer multiplexer_8 (.in0(F7), .in1(nF7), .out(MU7), .sel(D_I));  // open: en
  Multiplexer multiplexer_9 (.in0(F8), .in1(nF8), .out(MU8), .sel(D_I));  // open: en
  Multiplexer multiplexer_10 (.in0(F9), .in1(nF9), .out(MU9), .sel(D_I));  // open: en
  Multiplexer multiplexer_11 (.in0(F10), .in1(nF10), .out(MU10), .sel(D_I));  // open: en

  // Notes on the sheet:
  //   if /sum 1 reset latch
  //   if /sum 0 preset latch
endmodule

module Barrelshifter (
  input  MUI0,
  input  MUI1,
  input  MUI2,
  input  MUI3,
  input  MUI4,
  input  MUI5,
  input  MUI6,
  input  MUI7,
  input  MUI8,
  input  MUI9,
  input  MUI10,
  input  Dec_Inc,
  input  SR0,
  input  SR1,
  input  SR2,
  output S0,
  output S1,
  output S2,
  output S3,
  output S4,
  output S5,
  output S6,
  output S7,
  output S8,
  output S9,
  output S10
);

  wire multiplexer_1_out, multiplexer_2_out, multiplexer_3_out, multiplexer_4_out, multiplexer_5_out,
       multiplexer_6_out, multiplexer_7_out, multiplexer_8_out, multiplexer_9_out, multiplexer_10_out,
       multiplexer_11_out, multiplexer_12_out, multiplexer_13_out, multiplexer_14_out, multiplexer_15_out,
       multiplexer_16_out, multiplexer_17_out, multiplexer_18_out, multiplexer_19_out, multiplexer_20_out,
       multiplexer_21_out, multiplexer_22_out;

  Multiplexer multiplexer_1 (.in0(MUI0), .in1(MUI1), .out(multiplexer_1_out), .sel(SR0));  // open: en
  Multiplexer multiplexer_2 (.in0(MUI1), .in1(MUI2), .out(multiplexer_2_out), .sel(SR0));  // open: en
  Multiplexer multiplexer_3 (.in0(MUI2), .in1(MUI3), .out(multiplexer_3_out), .sel(SR0));  // open: en
  Multiplexer multiplexer_4 (.in0(MUI3), .in1(MUI4), .out(multiplexer_4_out), .sel(SR0));  // open: en
  Multiplexer multiplexer_5 (.in0(MUI4), .in1(MUI5), .out(multiplexer_5_out), .sel(SR0));  // open: en
  Multiplexer multiplexer_6 (.in0(MUI5), .in1(MUI6), .out(multiplexer_6_out), .sel(SR0));  // open: en
  Multiplexer multiplexer_7 (.in0(MUI6), .in1(MUI7), .out(multiplexer_7_out), .sel(SR0));  // open: en
  Multiplexer multiplexer_8 (.in0(MUI7), .in1(MUI8), .out(multiplexer_8_out), .sel(SR0));  // open: en
  Multiplexer multiplexer_9 (.in0(MUI8), .in1(MUI9), .out(multiplexer_9_out), .sel(SR0));  // open: en
  Multiplexer multiplexer_10 (.in0(MUI9), .in1(MUI10), .out(multiplexer_10_out), .sel(SR0));  // open: en
  Multiplexer multiplexer_11 (.in0(MUI10), .in1(Dec_Inc), .out(multiplexer_11_out), .sel(SR0));  // open: en
  Multiplexer multiplexer_12 (
    .in0(multiplexer_1_out), .in1(multiplexer_3_out), .out(multiplexer_12_out), .sel(SR1));  // open: en
  Multiplexer multiplexer_13 (
    .in0(multiplexer_2_out), .in1(multiplexer_4_out), .out(multiplexer_13_out), .sel(SR1));  // open: en
  Multiplexer multiplexer_14 (
    .in0(multiplexer_3_out), .in1(multiplexer_5_out), .out(multiplexer_14_out), .sel(SR1));  // open: en
  Multiplexer multiplexer_15 (
    .in0(multiplexer_4_out), .in1(multiplexer_6_out), .out(multiplexer_15_out), .sel(SR1));  // open: en
  Multiplexer multiplexer_16 (
    .in0(multiplexer_5_out), .in1(multiplexer_7_out), .out(multiplexer_16_out), .sel(SR1));  // open: en
  Multiplexer multiplexer_17 (
    .in0(multiplexer_6_out), .in1(multiplexer_8_out), .out(multiplexer_17_out), .sel(SR1));  // open: en
  Multiplexer multiplexer_18 (
    .in0(multiplexer_7_out), .in1(multiplexer_9_out), .out(multiplexer_18_out), .sel(SR1));  // open: en
  Multiplexer multiplexer_19 (
    .in0(multiplexer_8_out), .in1(multiplexer_10_out), .out(multiplexer_19_out), .sel(SR1));  // open: en
  Multiplexer multiplexer_20 (
    .in0(multiplexer_9_out), .in1(multiplexer_11_out), .out(multiplexer_20_out), .sel(SR1));  // open: en
  Multiplexer multiplexer_21 (
    .in0(multiplexer_10_out), .in1(Dec_Inc), .out(multiplexer_21_out), .sel(SR1));  // open: en
  Multiplexer multiplexer_22 (
    .in0(multiplexer_11_out), .in1(Dec_Inc), .out(multiplexer_22_out), .sel(SR1));  // open: en
  Multiplexer multiplexer_23 (.in0(multiplexer_12_out), .in1(multiplexer_16_out), .out(S0), .sel(SR2));  // open: en
  Multiplexer multiplexer_24 (.in0(multiplexer_13_out), .in1(multiplexer_17_out), .out(S1), .sel(SR2));  // open: en
  Multiplexer multiplexer_25 (.in0(multiplexer_14_out), .in1(multiplexer_18_out), .out(S2), .sel(SR2));  // open: en
  Multiplexer multiplexer_26 (.in0(multiplexer_15_out), .in1(multiplexer_19_out), .out(S3), .sel(SR2));  // open: en
  Multiplexer multiplexer_27 (.in0(multiplexer_16_out), .in1(multiplexer_20_out), .out(S4), .sel(SR2));  // open: en
  Multiplexer multiplexer_28 (.in0(multiplexer_17_out), .in1(multiplexer_21_out), .out(S5), .sel(SR2));  // open: en
  Multiplexer multiplexer_29 (.in0(multiplexer_18_out), .in1(multiplexer_22_out), .out(S6), .sel(SR2));  // open: en
  Multiplexer multiplexer_30 (.in0(multiplexer_19_out), .in1(Dec_Inc), .out(S7), .sel(SR2));  // open: en
  Multiplexer multiplexer_31 (.in0(multiplexer_20_out), .in1(Dec_Inc), .out(S8), .sel(SR2));  // open: en
  Multiplexer multiplexer_32 (.in0(multiplexer_21_out), .in1(Dec_Inc), .out(S9), .sel(SR2));  // open: en
  Multiplexer multiplexer_33 (.in0(multiplexer_22_out), .in1(Dec_Inc), .out(S10), .sel(SR2));  // open: en

  // Notes on the sheet:
  //   S0
  //   S1
  //   S2
  //   S3
  //   S4
  //   S5
  //   S6
  //   S7
  //   S8
  //   S9
  //   S10
endmodule

module Addercell (
  input  nCX,
  input  FX,
  input  nFX,
  input  SX,
  output FX_2,
  output nSum,
  output nCarryOut
);

  wire and_1_out, and_2_out, and_3_out, and_4_out, and_5_out, and_6_out, and_7_out, not_1_out, not_2_out;

  not not_1 (not_1_out, nCX);
  not not_2 (not_2_out, SX);
  and and_1 (and_1_out, not_2_out, not_1_out, FX);
  and and_2 (and_2_out, SX, FX);
  nor nor_1 (nCarryOut, and_2_out, and_1_out, and_3_out);
  and and_3 (and_3_out, SX, nFX, not_1_out);
  and and_4 (and_4_out, SX, nFX, nCX);
  and and_5 (and_5_out, not_2_out, FX, nCX);
  and and_6 (and_6_out, not_2_out, nFX, not_1_out);
  and and_7 (and_7_out, SX, not_1_out, FX);
  nor nor_2 (nSum, and_5_out, and_4_out, and_6_out, and_7_out);

  assign FX_2 = FX;

  // Notes on the sheet:
  //   /CX
  //   CX
  //   /FX
  //   /SX
  //   SX
endmodule

module SweepControl (
  input  nACLK,
  input  ACLK,
  input  W4001,
  input  D0,
  input  D1,
  input  D2,
  input  D3,
  input  D4,
  input  D5,
  input  D6,
  input  D7,
  input  nLFO2,
  input  NOSQA,
  input  nCOUT,
  input  SWEEP,
  input  RES,
  output SR0,
  output SR1,
  output SR2,
  output D_I,
  output ADDOUT,
  output SWEEP_2,
  output SWCTRL
);

  wire and_1_out, and_2_out, and_3_out, and_4_out, and_5_out, and_6_out, and_7_out, d_ff_5_q, d_ff_6_q,
       d_ff_7_q, d_ff_8_qn, d_ff_9_q, d_ff_9_qn, d_ff_10_q, d_ff_10_qn, d_ff_11_q, d_ff_11_qn, d_ff_12_qn,
       d_ff_13_q, d_ff_14_qn, d_ff_15_qn, d_ff_16_qn, d_ff_17_qn, d_ff_18_q, multiplexer_1_out,
       multiplexer_2_out, multiplexer_3_out, nor_1_out, nor_3_out, nor_4_out, nor_5_out, nor_6_out,
       nor_7_out, nor_8_out, nor_9_out, nor_10_out, nor_11_out, not_1_out, not_2_out, not_3_out, not_4_out,
       not_5_out, not_6_out, not_7_out, or_1_out, or_2_out, or_3_out;

  and and_1 (and_1_out, ACLK, W4001);
  D_Flip_Flop #(.trigger("high")) d_ff_1 (.clk(and_1_out), .D(D0), .Q(SR0));  // open: Qn, preset, en, reset
  D_Flip_Flop #(.trigger("high")) d_ff_2 (.clk(and_1_out), .D(D1), .Q(SR1));  // open: Qn, preset, en, reset
  D_Flip_Flop #(.trigger("high")) d_ff_3 (.clk(and_1_out), .D(D2), .Q(SR2));  // open: Qn, preset, en, reset
  D_Flip_Flop #(.trigger("high")) d_ff_4 (.clk(and_1_out), .D(D3), .Q(D_I));  // open: Qn, preset, en, reset
  D_Flip_Flop #(.trigger("high")) d_ff_5 (.clk(and_1_out), .D(D4), .Q(d_ff_5_q));  // open: Qn, preset, en, reset
  D_Flip_Flop #(.trigger("high")) d_ff_6 (.clk(and_1_out), .D(D5), .Q(d_ff_6_q));  // open: Qn, preset, en, reset
  D_Flip_Flop #(.trigger("high")) d_ff_7 (.clk(and_1_out), .D(D6), .Q(d_ff_7_q));  // open: Qn, preset, en, reset
  D_Flip_Flop #(.trigger("high")) d_ff_8 (.clk(and_1_out), .D(D7), .Qn(d_ff_8_qn));  // open: Q, preset, en, reset
  nor nor_1 (nor_1_out, nLFO2, d_ff_13_q);
  nor nor_2 (SWCTRL, D_I, nCOUT);
  and and_2 (and_2_out, d_ff_5_q, nor_7_out);
  not not_1 (not_1_out, d_ff_5_q);
  and and_3 (and_3_out, not_1_out, nor_7_out);
  and and_4 (and_4_out, d_ff_6_q, nor_7_out);
  not not_2 (not_2_out, d_ff_6_q);
  and and_5 (and_5_out, not_2_out, nor_7_out);
  and and_6 (and_6_out, d_ff_7_q, nor_7_out);
  not not_3 (not_3_out, d_ff_7_q);
  and and_7 (and_7_out, not_3_out, nor_7_out);
  nor nor_3 (nor_3_out, d_ff_18_q, d_ff_12_qn);
  nor nor_4 (nor_4_out, nor_1_out, nor_5_out);
  nor nor_5 (nor_5_out, nor_4_out, W4001);
  nor nor_6 (nor_6_out, SR0, SR1, SR2);
  D_Flip_Flop d_ff_9 (
    .clk(nor_8_out), .D(d_ff_14_qn), .Q(d_ff_9_q), .Qn(d_ff_9_qn), .preset(and_2_out), .reset(or_1_out));  // open: en
  or or_1 (or_1_out, and_3_out, RES);
  D_Flip_Flop d_ff_10 (
    .clk(nor_8_out), .D(d_ff_15_qn), .Q(d_ff_10_q), .Qn(d_ff_10_qn), .preset(and_4_out), .reset(or_2_out));  // open: en
  or or_2 (or_2_out, and_5_out, RES);
  D_Flip_Flop d_ff_11 (
    .clk(nor_8_out), .D(d_ff_16_qn), .Q(d_ff_11_q), .Qn(d_ff_11_qn), .preset(and_6_out), .reset(or_3_out));  // open: en
  or or_3 (or_3_out, and_7_out, RES);
  nor nor_7 (nor_7_out, nor_3_out, nLFO2);
  not not_4 (not_4_out, nor_3_out);
  Multiplexer multiplexer_1 (.in0(d_ff_9_qn), .in1(d_ff_9_q), .out(multiplexer_1_out), .sel(1'b1));  // open: en
  not not_5 (not_5_out, 1'b1);
  Multiplexer multiplexer_2 (.in0(d_ff_10_qn), .in1(d_ff_10_q), .out(multiplexer_2_out), .sel(nor_9_out));  // open: en
  not not_6 (not_6_out, nor_9_out);
  Multiplexer multiplexer_3 (.in0(d_ff_11_qn), .in1(d_ff_11_q), .out(multiplexer_3_out), .sel(nor_10_out));  // open: en
  not not_7 (not_7_out, nor_10_out);
  nor nor_8 (nor_8_out, not_4_out, nLFO2);
  D_Flip_Flop d_ff_12 (.clk(nACLK), .D(nor_5_out), .Qn(d_ff_12_qn));  // open: Q, preset, en, reset
  D_Flip_Flop d_ff_13 (.clk(nACLK), .Q(d_ff_13_q));  // open: D, Qn, preset, en, reset
  D_Flip_Flop d_ff_14 (.clk(nACLK), .D(multiplexer_1_out), .Qn(d_ff_14_qn));  // open: Q, preset, en, reset
  D_Flip_Flop d_ff_15 (.clk(nACLK), .D(multiplexer_2_out), .Qn(d_ff_15_qn));  // open: Q, preset, en, reset
  D_Flip_Flop d_ff_16 (.clk(nACLK), .D(multiplexer_3_out), .Qn(d_ff_16_qn));  // open: Q, preset, en, reset
  nor nor_9 (nor_9_out, d_ff_9_q, not_5_out);
  nor nor_10 (nor_10_out, d_ff_10_q, not_6_out);
  nor nor_11 (nor_11_out, d_ff_11_q, not_7_out);
  D_Flip_Flop d_ff_17 (.clk(nACLK), .D(nor_11_out), .Qn(d_ff_17_qn));  // open: Q, preset, en, reset
  D_Flip_Flop d_ff_18 (.clk(nACLK), .D(nor_11_out), .Q(d_ff_18_q));  // open: Qn, preset, en, reset
  nor nor_12 (ADDOUT, nor_6_out, d_ff_8_qn, NOSQA, SWCTRL, d_ff_17_qn, SWEEP, nLFO2);

  assign SWEEP_2 = SWEEP;

  // Notes on the sheet:
  //   SR0
  //   SR1
  //   SR2
  //   DEC/INC
  //   P0
  //   P1
  //   P2
  //   SWDIS
  //   SWEEPRELOAD
  //   NOR2
  //   NOR7
  //   NOR3
  //   NOR1
  //   NOR6
  //   INV1
  //   NORFF1
  //   RS1
  //   NORFF2
  //   NOR5
  //   DL1
  //   DL2
  //   DL3
  //   NOR4
endmodule

module Divider (
  input  nACLK,
  input  ACLK,
  input  W4000,
  input  W4003,
  input  RES,
  input  PL0,
  input  PL1,
  input  PL2,
  input  PL3,
  input  PL4,
  input  PL5,
  input  PL6,
  input  PL7,
  input  PL8,
  input  PL9,
  input  PL10,
  input  D6,
  input  D7,
  output FLOAD,
  output SQOUT
);

  wire and_1_out, and_2_out, and_3_out, and_4_out, and_5_out, and_6_out, and_7_out, and_8_out, and_9_out,
       and_10_out, and_11_out, and_12_out, and_13_out, and_14_out, and_15_out, and_16_out, and_17_out,
       and_18_out, and_19_out, and_20_out, and_21_out, and_22_out, and_23_out, d_ff_1_q, d_ff_1_qn, d_ff_2_q,
       d_ff_2_qn, d_ff_3_q, d_ff_3_qn, d_ff_4_q, d_ff_4_qn, d_ff_5_q, d_ff_5_qn, d_ff_6_q, d_ff_6_qn,
       d_ff_7_q, d_ff_7_qn, d_ff_8_q, d_ff_8_qn, d_ff_9_q, d_ff_9_qn, d_ff_10_q, d_ff_10_qn, d_ff_11_q,
       d_ff_11_qn, d_ff_12_q, d_ff_12_qn, d_ff_13_q, d_ff_13_qn, d_ff_14_q, d_ff_14_qn, d_ff_17_qn,
       d_ff_18_qn, d_ff_19_qn, d_ff_20_qn, d_ff_21_qn, d_ff_22_qn, d_ff_23_qn, d_ff_24_qn, d_ff_25_qn,
       d_ff_26_qn, d_ff_27_qn, d_ff_28_qn, d_ff_29_qn, d_ff_30_qn, d_ff_31_qn, multiplexer_1_out,
       multiplexer_2_out, multiplexer_3_out, multiplexer_4_out, multiplexer_5_out, multiplexer_6_out,
       multiplexer_7_out, multiplexer_8_out, multiplexer_9_out, multiplexer_10_out, multiplexer_11_out,
       multiplexer_12_out, multiplexer_13_out, multiplexer_14_out, nand_1_out, nor_2_out, nor_3_out,
       nor_4_out, nor_5_out, nor_6_out, nor_7_out, nor_8_out, nor_9_out, nor_10_out, nor_11_out, nor_12_out,
       nor_13_out, nor_14_out, nor_15_out, nor_16_out, not_1_out, not_2_out, not_3_out, not_4_out, not_5_out,
       not_6_out, not_7_out, not_8_out, not_9_out, not_10_out, not_11_out, not_12_out, not_13_out,
       not_14_out, not_15_out, not_16_out, not_17_out, not_18_out, not_19_out, not_20_out, not_21_out,
       not_22_out, not_23_out, not_24_out, not_25_out, not_26_out, not_27_out, or_1_out, or_2_out, or_3_out,
       or_4_out, or_5_out, or_6_out, or_7_out, or_8_out, or_9_out, or_10_out, or_11_out, or_12_out,
       or_13_out, or_14_out;
  wire [1:0] d_ff_15_q;
  wire [13:0] counter_1_q, register_1_q;

  Counter #(.width(14), .max('h3fff)) counter_1 (
    .Q(counter_1_q), .clk(nor_2_out), .clr(FLOAD));  // open: load, D, count, carry
  not not_1 (not_1_out, PL0);
  not not_2 (not_2_out, PL1);
  not not_3 (not_3_out, PL2);
  not not_4 (not_4_out, PL3);
  not not_5 (not_5_out, PL4);
  not not_6 (not_6_out, PL5);
  not not_7 (not_7_out, PL6);
  not not_8 (not_8_out, PL7);
  not not_9 (not_9_out, PL8);
  not not_10 (not_10_out, PL9);
  not not_11 (not_11_out, PL10);
  Register #(.width(14)) register_1 (.D(counter_1_q), .Q(register_1_q), .clk(FLOAD));  // open: en, clr
  D_Flip_Flop d_ff_1 (
    .clk(nor_2_out), .D(d_ff_17_qn), .Q(d_ff_1_q), .Qn(d_ff_1_qn), .preset(and_1_out), .reset(or_1_out));  // open: en
  and and_1 (and_1_out, FLOAD, PL0);
  and and_2 (and_2_out, FLOAD, not_1_out);
  or or_1 (or_1_out, and_2_out, RES);
  D_Flip_Flop d_ff_2 (
    .clk(nor_2_out), .D(d_ff_18_qn), .Q(d_ff_2_q), .Qn(d_ff_2_qn), .preset(and_3_out), .reset(or_2_out));  // open: en
  and and_3 (and_3_out, FLOAD, PL1);
  and and_4 (and_4_out, FLOAD, not_2_out);
  or or_2 (or_2_out, and_4_out, RES);
  D_Flip_Flop d_ff_3 (
    .clk(nor_2_out), .D(d_ff_19_qn), .Q(d_ff_3_q), .Qn(d_ff_3_qn), .preset(and_5_out), .reset(or_3_out));  // open: en
  and and_5 (and_5_out, FLOAD, PL2);
  and and_6 (and_6_out, FLOAD, not_3_out);
  or or_3 (or_3_out, and_6_out, RES);
  D_Flip_Flop d_ff_4 (
    .clk(nor_2_out), .D(d_ff_20_qn), .Q(d_ff_4_q), .Qn(d_ff_4_qn), .preset(and_7_out), .reset(or_4_out));  // open: en
  and and_7 (and_7_out, FLOAD, PL3);
  and and_8 (and_8_out, FLOAD, not_4_out);
  or or_4 (or_4_out, and_8_out, RES);
  D_Flip_Flop d_ff_5 (
    .clk(nor_2_out), .D(d_ff_21_qn), .Q(d_ff_5_q), .Qn(d_ff_5_qn), .preset(and_9_out), .reset(or_5_out));  // open: en
  and and_9 (and_9_out, FLOAD, PL4);
  and and_10 (and_10_out, FLOAD, not_5_out);
  or or_5 (or_5_out, and_10_out, RES);
  D_Flip_Flop d_ff_6 (
    .clk(nor_2_out), .D(d_ff_22_qn), .Q(d_ff_6_q), .Qn(d_ff_6_qn), .preset(and_11_out), .reset(or_6_out));  // open: en
  and and_11 (and_11_out, FLOAD, PL5);
  and and_12 (and_12_out, FLOAD, not_6_out);
  or or_6 (or_6_out, and_12_out, RES);
  D_Flip_Flop d_ff_7 (
    .clk(nor_2_out), .D(d_ff_23_qn), .Q(d_ff_7_q), .Qn(d_ff_7_qn), .preset(and_13_out), .reset(or_7_out));  // open: en
  and and_13 (and_13_out, FLOAD, PL6);
  and and_14 (and_14_out, FLOAD, not_7_out);
  or or_7 (or_7_out, and_14_out, RES);
  D_Flip_Flop d_ff_8 (
    .clk(nor_2_out), .D(d_ff_24_qn), .Q(d_ff_8_q), .Qn(d_ff_8_qn), .preset(and_15_out), .reset(or_8_out));  // open: en
  and and_15 (and_15_out, FLOAD, PL7);
  and and_16 (and_16_out, FLOAD, not_8_out);
  or or_8 (or_8_out, and_16_out, RES);
  D_Flip_Flop d_ff_9 (
    .clk(nor_2_out), .D(d_ff_25_qn), .Q(d_ff_9_q), .Qn(d_ff_9_qn), .preset(and_17_out), .reset(or_9_out));  // open: en
  and and_17 (and_17_out, FLOAD, PL8);
  and and_18 (and_18_out, FLOAD, not_9_out);
  or or_9 (or_9_out, and_18_out, RES);
  D_Flip_Flop d_ff_10 (
    .clk(nor_2_out), .D(d_ff_26_qn), .Q(d_ff_10_q), .Qn(d_ff_10_qn), .preset(and_19_out), .reset(or_10_out));  // open: en
  and and_19 (and_19_out, FLOAD, PL9);
  and and_20 (and_20_out, FLOAD, not_10_out);
  or or_10 (or_10_out, and_20_out, RES);
  D_Flip_Flop d_ff_11 (
    .clk(nor_2_out), .D(d_ff_27_qn), .Q(d_ff_11_q), .Qn(d_ff_11_qn), .preset(and_21_out), .reset(or_11_out));  // open: en
  and and_21 (and_21_out, FLOAD, PL10);
  and and_22 (and_22_out, FLOAD, not_11_out);
  or or_11 (or_11_out, and_22_out, RES);
  // Probe on register_1_q
  D_Flip_Flop d_ff_12 (
    .clk(FLOAD), .D(d_ff_28_qn), .Q(d_ff_12_q), .Qn(d_ff_12_qn), .reset(or_12_out));  // open: preset, en
  or or_12 (or_12_out, W4003, RES);
  D_Flip_Flop d_ff_13 (
    .clk(FLOAD), .D(d_ff_29_qn), .Q(d_ff_13_q), .Qn(d_ff_13_qn), .reset(or_13_out));  // open: preset, en
  or or_13 (or_13_out, W4003, RES);
  D_Flip_Flop d_ff_14 (
    .clk(FLOAD), .D(d_ff_30_qn), .Q(d_ff_14_q), .Qn(d_ff_14_qn), .reset(or_14_out));  // open: preset, en
  or or_14 (or_14_out, W4003, RES);
  and and_23 (and_23_out, ACLK, W4000);
  D_Flip_Flop #(.trigger("high")) d_ff_15 (.clk(and_23_out), .D(D6), .Q(d_ff_15_q[0]));  // open: Qn, preset, en, reset
  D_Flip_Flop #(.trigger("high")) d_ff_16 (.clk(and_23_out), .D(D7), .Q(d_ff_15_q[1]));  // open: Qn, preset, en, reset
  Multiplexer multiplexer_1 (.in0(d_ff_1_qn), .in1(d_ff_1_q), .out(multiplexer_1_out), .sel(1'b1));  // open: en
  Multiplexer multiplexer_2 (.in0(d_ff_2_qn), .in1(d_ff_2_q), .out(multiplexer_2_out), .sel(nor_3_out));  // open: en
  Multiplexer multiplexer_3 (.in0(d_ff_3_qn), .in1(d_ff_3_q), .out(multiplexer_3_out), .sel(nor_4_out));  // open: en
  Multiplexer multiplexer_4 (.in0(d_ff_4_qn), .in1(d_ff_4_q), .out(multiplexer_4_out), .sel(nor_5_out));  // open: en
  Multiplexer multiplexer_5 (.in0(d_ff_5_qn), .in1(d_ff_5_q), .out(multiplexer_5_out), .sel(nor_6_out));  // open: en
  Multiplexer multiplexer_6 (.in0(d_ff_6_qn), .in1(d_ff_6_q), .out(multiplexer_6_out), .sel(nor_7_out));  // open: en
  Multiplexer multiplexer_7 (.in0(d_ff_7_qn), .in1(d_ff_7_q), .out(multiplexer_7_out), .sel(nor_8_out));  // open: en
  Multiplexer multiplexer_8 (.in0(d_ff_8_qn), .in1(d_ff_8_q), .out(multiplexer_8_out), .sel(nor_9_out));  // open: en
  Multiplexer multiplexer_9 (.in0(d_ff_9_qn), .in1(d_ff_9_q), .out(multiplexer_9_out), .sel(nor_10_out));  // open: en
  Multiplexer multiplexer_10 (
    .in0(d_ff_10_qn), .in1(d_ff_10_q), .out(multiplexer_10_out), .sel(nor_11_out));  // open: en
  Multiplexer multiplexer_11 (
    .in0(d_ff_11_qn), .in1(d_ff_11_q), .out(multiplexer_11_out), .sel(nor_12_out));  // open: en
  nor nor_1 (FLOAD, d_ff_31_qn, nACLK);
  nor nor_2 (nor_2_out, nACLK, not_23_out);
  Multiplexer multiplexer_12 (
    .in0(d_ff_12_qn), .in1(d_ff_12_q), .out(multiplexer_12_out), .sel(nor_13_out));  // open: en
  Multiplexer multiplexer_13 (
    .in0(d_ff_13_qn), .in1(d_ff_13_q), .out(multiplexer_13_out), .sel(nor_14_out));  // open: en
  Multiplexer multiplexer_14 (
    .in0(d_ff_14_qn), .in1(d_ff_14_q), .out(multiplexer_14_out), .sel(nor_15_out));  // open: en
  D_Flip_Flop #(.trigger("high")) d_ff_17 (
    .clk(nACLK), .D(multiplexer_1_out), .Qn(d_ff_17_qn));  // open: Q, preset, en, reset
  not not_12 (not_12_out, 1'b1);
  D_Flip_Flop #(.trigger("high")) d_ff_18 (
    .clk(nACLK), .D(multiplexer_2_out), .Qn(d_ff_18_qn));  // open: Q, preset, en, reset
  not not_13 (not_13_out, nor_3_out);
  D_Flip_Flop #(.trigger("high")) d_ff_19 (
    .clk(nACLK), .D(multiplexer_3_out), .Qn(d_ff_19_qn));  // open: Q, preset, en, reset
  not not_14 (not_14_out, nor_4_out);
  D_Flip_Flop #(.trigger("high")) d_ff_20 (
    .clk(nACLK), .D(multiplexer_4_out), .Qn(d_ff_20_qn));  // open: Q, preset, en, reset
  not not_15 (not_15_out, nor_5_out);
  D_Flip_Flop #(.trigger("high")) d_ff_21 (
    .clk(nACLK), .D(multiplexer_5_out), .Qn(d_ff_21_qn));  // open: Q, preset, en, reset
  not not_16 (not_16_out, nor_6_out);
  D_Flip_Flop #(.trigger("high")) d_ff_22 (
    .clk(nACLK), .D(multiplexer_6_out), .Qn(d_ff_22_qn));  // open: Q, preset, en, reset
  not not_17 (not_17_out, nor_7_out);
  D_Flip_Flop #(.trigger("high")) d_ff_23 (
    .clk(nACLK), .D(multiplexer_7_out), .Qn(d_ff_23_qn));  // open: Q, preset, en, reset
  not not_18 (not_18_out, nor_8_out);
  D_Flip_Flop #(.trigger("high")) d_ff_24 (
    .clk(nACLK), .D(multiplexer_8_out), .Qn(d_ff_24_qn));  // open: Q, preset, en, reset
  not not_19 (not_19_out, nor_9_out);
  D_Flip_Flop #(.trigger("high")) d_ff_25 (
    .clk(nACLK), .D(multiplexer_9_out), .Qn(d_ff_25_qn));  // open: Q, preset, en, reset
  not not_20 (not_20_out, nor_10_out);
  D_Flip_Flop #(.trigger("high")) d_ff_26 (
    .clk(nACLK), .D(multiplexer_10_out), .Qn(d_ff_26_qn));  // open: Q, preset, en, reset
  not not_21 (not_21_out, nor_11_out);
  D_Flip_Flop #(.trigger("high")) d_ff_27 (
    .clk(nACLK), .D(multiplexer_11_out), .Qn(d_ff_27_qn));  // open: Q, preset, en, reset
  not not_22 (not_22_out, nor_12_out);
  not not_23 (not_23_out, d_ff_31_qn);
  D_Flip_Flop d_ff_28 (.clk(nACLK), .D(multiplexer_12_out), .Qn(d_ff_28_qn));  // open: Q, preset, en, reset
  not not_24 (not_24_out, nor_13_out);
  D_Flip_Flop d_ff_29 (.clk(nACLK), .D(multiplexer_13_out), .Qn(d_ff_29_qn));  // open: Q, preset, en, reset
  not not_25 (not_25_out, nor_14_out);
  D_Flip_Flop d_ff_30 (.clk(nACLK), .D(multiplexer_14_out), .Qn(d_ff_30_qn));  // open: Q, preset, en, reset
  nor nor_3 (nor_3_out, d_ff_1_q, not_12_out);
  nor nor_4 (nor_4_out, d_ff_2_q, not_13_out);
  nor nor_5 (nor_5_out, d_ff_3_q, not_14_out);
  nor nor_6 (nor_6_out, d_ff_4_q, not_15_out);
  nor nor_7 (nor_7_out, d_ff_5_q, not_16_out);
  nor nor_8 (nor_8_out, d_ff_6_q, not_17_out);
  nor nor_9 (nor_9_out, d_ff_7_q, not_18_out);
  nor nor_10 (nor_10_out, d_ff_8_q, not_19_out);
  nor nor_11 (nor_11_out, d_ff_9_q, not_20_out);
  nor nor_12 (nor_12_out, d_ff_10_q, not_21_out);
  nor nor_13 (nor_13_out, d_ff_11_q, not_22_out);
  nor nor_14 (nor_14_out, d_ff_12_q, not_24_out);
  nor nor_15 (nor_15_out, d_ff_13_q, not_25_out);
  not not_26 (not_26_out, d_ff_12_q);
  D_Flip_Flop d_ff_31 (.clk(nACLK), .D(nor_13_out), .Qn(d_ff_31_qn));  // open: Q, preset, en, reset
  nor nor_16 (nor_16_out, not_26_out, nand_1_out);
  not not_27 (not_27_out, nand_1_out);
  nand nand_1 (nand_1_out, d_ff_13_q, d_ff_14_q);
  Multiplexer #(.select(2)) multiplexer_15 (
    .in0(nor_16_out), .in1(not_27_out), .in2(d_ff_14_q), .in3(nand_1_out), .out(SQOUT), .sel(d_ff_15_q));  // open: en

  // Notes on the sheet:
  //   FLOAD
  //   NOR8
  //   STEP
  //   INV2
  //   DL4
  //   INV3
  //   NOR10
  //   INV4
  //   NAND1
  //   50%
  //   12.5%
  //   25%
  //   75%
endmodule

module Envelope_Generator (
  input  nACLK,
  input  ACLK,
  input  W4000,
  input  W4003,
  input  D0,
  input  D1,
  input  D2,
  input  D3,
  input  D4,
  input  D5,
  input  nLFO1,
  input  RES,
  output VOL0,
  output VOL1,
  output VOL2,
  output VOL3,
  output ENVDIS,
  output Env0,
  output Env1,
  output Env2,
  output Env3
);

  wire and_1_out, and_2_out, and_3_out, and_4_out, and_5_out, and_6_out, and_7_out, and_8_out, and_9_out,
       and_10_out, and_11_out, and_12_out, and_13_out, and_14_out, and_15_out, and_16_out, and_17_out,
       d_ff_6_qn, d_ff_7_qn, d_ff_8_q, d_ff_9_q, d_ff_10_q, d_ff_11_q, d_ff_12_q, d_ff_12_qn, d_ff_13_q,
       d_ff_13_qn, d_ff_14_q, d_ff_14_qn, d_ff_15_q, d_ff_15_qn, d_ff_16_q, d_ff_17_qn, d_ff_18_qn,
       d_ff_19_qn, d_ff_20_qn, d_ff_21_qn, d_ff_22_qn, d_ff_23_qn, d_ff_24_qn, d_ff_25_qn, d_ff_26_qn,
       d_ff_27_qn, d_ff_28_qn, multiplexer_1_out, multiplexer_2_out, multiplexer_3_out, multiplexer_4_out,
       multiplexer_5_out, multiplexer_6_out, multiplexer_7_out, multiplexer_8_out, nand_1_out, nor_1_out,
       nor_2_out, nor_3_out, nor_4_out, nor_5_out, nor_6_out, nor_7_out, nor_8_out, nor_9_out, nor_10_out,
       nor_11_out, nor_12_out, nor_13_out, nor_14_out, nor_15_out, nor_16_out, nor_17_out, not_1_out,
       not_2_out, not_3_out, not_4_out, not_5_out, not_6_out, not_7_out, not_8_out, not_9_out, not_10_out,
       not_11_out, not_12_out, not_13_out, not_14_out, not_15_out, not_16_out, not_17_out, not_18_out,
       or_1_out, or_2_out, or_3_out, or_4_out, or_5_out, or_6_out, or_7_out, or_8_out;

  and and_1 (and_1_out, ACLK, W4000);
  D_Flip_Flop #(.trigger("high")) d_ff_1 (.clk(and_1_out), .D(D0), .Q(VOL0));  // open: Qn, preset, en, reset
  D_Flip_Flop #(.trigger("high")) d_ff_2 (.clk(and_1_out), .D(D1), .Q(VOL1));  // open: Qn, preset, en, reset
  D_Flip_Flop #(.trigger("high")) d_ff_3 (.clk(and_1_out), .D(D2), .Q(VOL2));  // open: Qn, preset, en, reset
  D_Flip_Flop #(.trigger("high")) d_ff_4 (.clk(and_1_out), .D(D3), .Q(VOL3));  // open: Qn, preset, en, reset
  D_Flip_Flop #(.trigger("high")) d_ff_5 (.clk(and_1_out), .D(D4), .Q(ENVDIS));  // open: Qn, preset, en, reset
  D_Flip_Flop #(.trigger("high")) d_ff_6 (.clk(and_1_out), .D(D5), .Qn(d_ff_6_qn));  // open: Q, preset, en, reset
  nor nor_1 (nor_1_out, nor_13_out, nor_2_out);
  not not_1 (not_1_out, VOL0);
  not not_2 (not_2_out, VOL1);
  not not_3 (not_3_out, VOL2);
  not not_4 (not_4_out, VOL3);
  D_Flip_Flop d_ff_7 (.clk(nACLK), .D(nor_1_out), .Qn(d_ff_7_qn));  // open: Q, preset, en, reset
  D_Flip_Flop d_ff_8 (.clk(nACLK), .D(nor_1_out), .Q(d_ff_8_q));  // open: Qn, preset, en, reset
  not not_5 (not_5_out, nand_1_out);
  not not_6 (not_6_out, nand_1_out);
  not not_7 (not_7_out, nand_1_out);
  not not_8 (not_8_out, nand_1_out);
  D_Flip_Flop d_ff_9 (.clk(nACLK), .D(nor_17_out), .Q(d_ff_9_q));  // open: Qn, preset, en, reset
  D_Flip_Flop d_ff_10 (.clk(nACLK), .D(nor_17_out), .Q(d_ff_10_q));  // open: Qn, preset, en, reset
  D_Flip_Flop d_ff_11 (.clk(nACLK), .D(nor_2_out), .Q(d_ff_11_q));  // open: Qn, preset, en, reset
  and and_2 (and_2_out, VOL0, nor_5_out);
  and and_3 (and_3_out, not_1_out, nor_5_out);
  and and_4 (and_4_out, VOL1, nor_5_out);
  and and_5 (and_5_out, not_2_out, nor_5_out);
  and and_6 (and_6_out, VOL2, nor_5_out);
  and and_7 (and_7_out, not_3_out, nor_5_out);
  and and_8 (and_8_out, VOL3, nor_5_out);
  and and_9 (and_9_out, not_4_out, nor_5_out);
  nor nor_2 (nor_2_out, nor_7_out, nor_3_out);
  nor nor_3 (nor_3_out, nor_2_out, W4003);
  nor nor_4 (nor_4_out, d_ff_7_qn, nLFO1);
  nor nor_5 (nor_5_out, d_ff_8_q, nLFO1);
  and and_10 (and_10_out, nand_1_out, nor_9_out);
  and and_11 (and_11_out, not_5_out, nor_9_out);
  and and_12 (and_12_out, nand_1_out, nor_9_out);
  and and_13 (and_13_out, not_6_out, nor_9_out);
  and and_14 (and_14_out, nand_1_out, nor_9_out);
  and and_15 (and_15_out, not_7_out, nor_9_out);
  and and_16 (and_16_out, nand_1_out, nor_9_out);
  and and_17 (and_17_out, not_8_out, nor_9_out);
  nand nand_1 (nand_1_out, d_ff_9_q, d_ff_6_qn);
  nor nor_6 (nor_6_out, d_ff_10_q, d_ff_11_q);
  D_Flip_Flop d_ff_12 (
    .clk(nor_4_out), .D(d_ff_21_qn), .Q(d_ff_12_q), .Qn(d_ff_12_qn), .preset(and_2_out), .reset(or_1_out));  // open: en
  or or_1 (or_1_out, and_3_out, RES);
  D_Flip_Flop d_ff_13 (
    .clk(nor_4_out), .D(d_ff_22_qn), .Q(d_ff_13_q), .Qn(d_ff_13_qn), .preset(and_4_out), .reset(or_2_out));  // open: en
  or or_2 (or_2_out, and_5_out, RES);
  D_Flip_Flop d_ff_14 (
    .clk(nor_4_out), .D(d_ff_23_qn), .Q(d_ff_14_q), .Qn(d_ff_14_qn), .preset(and_6_out), .reset(or_3_out));  // open: en
  or or_3 (or_3_out, and_7_out, RES);
  D_Flip_Flop d_ff_15 (
    .clk(nor_4_out), .D(d_ff_24_qn), .Q(d_ff_15_q), .Qn(d_ff_15_qn), .preset(and_8_out), .reset(or_4_out));  // open: en
  or or_4 (or_4_out, and_9_out, RES);
  D_Flip_Flop d_ff_16 (.clk(nACLK), .D(nor_3_out), .Q(d_ff_16_q));  // open: Qn, preset, en, reset
  D_Flip_Flop d_ff_17 (
    .clk(nor_8_out), .D(d_ff_25_qn), .Q(Env0), .Qn(d_ff_17_qn), .preset(and_10_out), .reset(or_5_out));  // open: en
  or or_5 (or_5_out, and_11_out, RES);
  D_Flip_Flop d_ff_18 (
    .clk(nor_8_out), .D(d_ff_26_qn), .Q(Env1), .Qn(d_ff_18_qn), .preset(and_12_out), .reset(or_6_out));  // open: en
  or or_6 (or_6_out, and_13_out, RES);
  D_Flip_Flop d_ff_19 (
    .clk(nor_8_out), .D(d_ff_27_qn), .Q(Env2), .Qn(d_ff_19_qn), .preset(and_14_out), .reset(or_7_out));  // open: en
  or or_7 (or_7_out, and_15_out, RES);
  D_Flip_Flop d_ff_20 (
    .clk(nor_8_out), .D(d_ff_28_qn), .Q(Env3), .Qn(d_ff_20_qn), .preset(and_16_out), .reset(or_8_out));  // open: en
  or or_8 (or_8_out, and_17_out, RES);
  not not_9 (not_9_out, nor_5_out);
  not not_10 (not_10_out, nor_6_out);
  Multiplexer multiplexer_1 (.in0(d_ff_12_qn), .in1(d_ff_12_q), .out(multiplexer_1_out), .sel(1'b1));  // open: en
  not not_11 (not_11_out, 1'b1);
  Multiplexer multiplexer_2 (.in0(d_ff_13_qn), .in1(d_ff_13_q), .out(multiplexer_2_out), .sel(nor_10_out));  // open: en
  not not_12 (not_12_out, nor_10_out);
  Multiplexer multiplexer_3 (.in0(d_ff_14_qn), .in1(d_ff_14_q), .out(multiplexer_3_out), .sel(nor_11_out));  // open: en
  not not_13 (not_13_out, nor_11_out);
  Multiplexer multiplexer_4 (.in0(d_ff_15_qn), .in1(d_ff_15_q), .out(multiplexer_4_out), .sel(nor_12_out));  // open: en
  not not_14 (not_14_out, nor_12_out);
  nor nor_7 (nor_7_out, d_ff_16_q, nLFO1);
  Multiplexer multiplexer_5 (.in0(d_ff_17_qn), .in1(Env0), .out(multiplexer_5_out), .sel(1'b1));  // open: en
  not not_15 (not_15_out, 1'b1);
  Multiplexer multiplexer_6 (.in0(d_ff_18_qn), .in1(Env1), .out(multiplexer_6_out), .sel(nor_14_out));  // open: en
  not not_16 (not_16_out, nor_14_out);
  Multiplexer multiplexer_7 (.in0(d_ff_19_qn), .in1(Env2), .out(multiplexer_7_out), .sel(nor_15_out));  // open: en
  not not_17 (not_17_out, nor_15_out);
  Multiplexer multiplexer_8 (.in0(d_ff_20_qn), .in1(Env3), .out(multiplexer_8_out), .sel(nor_16_out));  // open: en
  not not_18 (not_18_out, nor_16_out);
  nor nor_8 (nor_8_out, not_9_out, not_10_out);
  nor nor_9 (nor_9_out, not_9_out, nor_6_out);
  D_Flip_Flop d_ff_21 (.clk(nACLK), .D(multiplexer_1_out), .Qn(d_ff_21_qn));  // open: Q, preset, en, reset
  D_Flip_Flop d_ff_22 (.clk(nACLK), .D(multiplexer_2_out), .Qn(d_ff_22_qn));  // open: Q, preset, en, reset
  D_Flip_Flop d_ff_23 (.clk(nACLK), .D(multiplexer_3_out), .Qn(d_ff_23_qn));  // open: Q, preset, en, reset
  D_Flip_Flop d_ff_24 (.clk(nACLK), .D(multiplexer_4_out), .Qn(d_ff_24_qn));  // open: Q, preset, en, reset
  D_Flip_Flop d_ff_25 (.clk(nACLK), .D(multiplexer_5_out), .Qn(d_ff_25_qn));  // open: Q, preset, en, reset
  D_Flip_Flop d_ff_26 (.clk(nACLK), .D(multiplexer_6_out), .Qn(d_ff_26_qn));  // open: Q, preset, en, reset
  D_Flip_Flop d_ff_27 (.clk(nACLK), .D(multiplexer_7_out), .Qn(d_ff_27_qn));  // open: Q, preset, en, reset
  D_Flip_Flop d_ff_28 (.clk(nACLK), .D(multiplexer_8_out), .Qn(d_ff_28_qn));  // open: Q, preset, en, reset
  nor nor_10 (nor_10_out, d_ff_12_q, not_11_out);
  nor nor_11 (nor_11_out, d_ff_13_q, not_12_out);
  nor nor_12 (nor_12_out, d_ff_14_q, not_13_out);
  nor nor_13 (nor_13_out, d_ff_15_q, not_14_out);
  nor nor_14 (nor_14_out, Env0, not_15_out);
  nor nor_15 (nor_15_out, Env1, not_16_out);
  nor nor_16 (nor_16_out, Env2, not_17_out);
  nor nor_17 (nor_17_out, Env3, nor_2_out, not_18_out);

  // Notes on the sheet:
  //   ENDIS
  //   SQA/LC
  //   NOR17
  //   RS1
  //   NORFF2
  //   DL10
  //   DL11
  //   DL7
  //   DL8
  //   DL9
  //   NORFF1
  //   NOR16
  //   NOR15
  //   LOAD
  //   NAND2
  //   NOR18
  //   RELOAD
  //   DL6
  //   RSTEP
  //   INV6
  //   INV7
  //   NOR12
  //   ESTEP
  //   NOR19
  //   NOR14
  //   ERES
endmodule

module Masterclock (
  input  PHI0,
  input  RES,
  output PHI1,
  output PHI2,
  output ACLK,
  output nACLK
);

  wire d_ff_1_qn, d_ff_2_qn, nor_1_out, nor_2_out, not_2_out;

  not not_1 (PHI1, PHI0);
  not not_2 (not_2_out, PHI1);
  D_Flip_Flop d_ff_1 (.clk(PHI1), .D(nor_1_out), .Qn(d_ff_1_qn));  // open: Q, preset, en, reset
  D_Flip_Flop d_ff_2 (.clk(PHI0), .D(d_ff_1_qn), .Qn(d_ff_2_qn));  // open: Q, preset, en, reset
  nor nor_1 (nor_1_out, d_ff_2_qn, RES);
  nor nor_2 (nor_2_out, nor_1_out, not_2_out);
  nor nor_3 (nACLK, not_2_out, PHI0, d_ff_2_qn);
  not not_3 (ACLK, nor_2_out);

  assign PHI2 = PHI0;

  // Notes on the sheet:
  //   INV1
  //   DL1
  //   DL2
  //   NOR1
  //   NOR2
  //   NOR3
endmodule
