// Logisim project databuscontrol.circ as structural Verilog: 1 circuit, main circuit main
module main (
  input  [7:0] in_1,
  input  [7:0] in_2,
  input  [7:0] Data_from_cpu,
  input  nR4015,
  input  SPR_PPU,
  output [7:0] Data_to_CPU,
  output [7:0] APU_registers_and_sprite_buffer
);

  wire not_1_out, not_2_out, or_1_out;
  wire [7:0] multiplexer_1_out;

  not not_1 (not_1_out, nR4015);
  assign APU_registers_and_sprite_buffer = not_2_out ? Data_from_cpu : 8'bz;  // Controlled_Buffer controlled_buffer_1
  not not_2 (not_2_out, or_1_out);
  or or_1 (or_1_out, not_1_out, SPR_PPU);
  assign Data_to_CPU = or_1_out ? multiplexer_1_out : 8'bz;  // Controlled_Buffer controlled_buffer_2
  Multiplexer #(.width(8)) multiplexer_1 (.in0(in_1), .in1(in_2), .out(multiplexer_1_out), .sel(SPR_PPU));  // open: en

  // Notes on the sheet:
  //   (Output to databus)
  //   (Input from databus)
  //   Port 4015 read
  //   Sprite buffer read
endmodule
