// Logisim project datapad.circ as structural Verilog: 1 circuit, main circuit main
module main (
  input  data_internal_cpu,
  input  R_W,
  input  data_in__pad,
  output _1_data,
  output data_out__pad,
  output _0_data,
  output rd,
  output data_out_to_cpu_internal,
  output wd
);

  wire pull_resistor_1_node, pull_resistor_2_node, pull_resistor_3_node, pull_resistor_4_node,
       pull_resistor_7_node, pull_resistor_8_node, pull_resistor_10_node, transistor_10_out,
       transistor_12_out, transistor_16_out;

  not not_1 (wd, R_W);
  Pull_Resistor #(.pull(1)) pull_resistor_1 (.node(pull_resistor_1_node));
  Transistor #(.\type ("n")) transistor_1 (.in(1'b0), .out(pull_resistor_1_node), .gate(data_internal_cpu));
  Transistor #(.\type ("n")) transistor_2 (.in(1'b0), .out(pull_resistor_1_node), .gate(R_W));
  Pull_Resistor #(.pull(1)) pull_resistor_2 (.node(pull_resistor_2_node));
  Transistor #(.\type ("n"), .gate("br")) transistor_3 (
    .in(pull_resistor_2_node), .out(data_out_to_cpu_internal), .gate(transistor_10_out));
  Transistor #(.\type ("n"), .gate("br")) transistor_4 (
    .in(1'b0), .out(data_out_to_cpu_internal), .gate(transistor_16_out));
  Pull_Resistor #(.pull(1)) pull_resistor_3 (.node(pull_resistor_3_node));
  Transistor #(.\type ("n")) transistor_5 (.in(pull_resistor_3_node), .out(_0_data), .gate(pull_resistor_1_node));
  Transistor #(.\type ("n")) transistor_6 (.in(1'b0), .out(_0_data), .gate(R_W));
  Transistor #(.\type ("n")) transistor_7 (.in(1'b0), .out(_0_data), .gate(transistor_12_out));
  Pull_Resistor #(.pull(1)) pull_resistor_4 (.node(pull_resistor_4_node));
  Transistor #(.\type ("n"), .gate("br")) transistor_8 (
    .in(pull_resistor_4_node), .out(_1_data), .gate(transistor_12_out));
  Transistor #(.\type ("n")) transistor_9 (.in(1'b0), .out(_1_data), .gate(R_W));
  Transistor #(.\type ("n")) transistor_10 (.in(1'b0), .out(transistor_10_out), .gate(transistor_16_out));
  Transistor #(.\type ("n"), .gate("br")) transistor_11 (.in(1'b0), .out(_1_data), .gate(pull_resistor_1_node));
  Transistor #(.\type ("n")) transistor_12 (.in(1'b0), .out(transistor_12_out), .gate(pull_resistor_1_node));
  Pull_Resistor #(.pull(1)) pull_resistor_5 (.node(transistor_10_out));
  Transistor #(.\type ("n"), .gate("br")) transistor_13 (.in(1'b0), .out(transistor_10_out), .gate(transistor_16_out));
  Transistor #(.\type ("n")) transistor_14 (.in(1'b0), .out(transistor_10_out), .gate(wd));
  Pull_Resistor #(.pull(1)) pull_resistor_6 (.node(transistor_12_out));
  Transistor #(.\type ("n"), .gate("br")) transistor_15 (.in(1'b0), .out(transistor_12_out), .gate(R_W));
  Transistor #(.\type ("n")) transistor_16 (.in(1'b0), .out(transistor_16_out), .gate(wd));
  Pull_Resistor #(.pull(1)) pull_resistor_7 (.node(pull_resistor_7_node));
  Transistor #(.\type ("n")) transistor_17 (.in(pull_resistor_7_node), .out(data_out__pad), .gate(_1_data));
  Transistor #(.\type ("n")) transistor_18 (.in(1'b0), .out(data_out__pad), .gate(_0_data));
  Pull_Resistor #(.pull(1)) pull_resistor_8 (.node(pull_resistor_8_node));
  Pull_Resistor #(.pull(1)) pull_resistor_9 (.node(transistor_16_out));
  Transistor #(.\type ("n"), .gate("br")) transistor_19 (
    .in(1'b0), .out(pull_resistor_8_node), .gate(pull_resistor_10_node));
  Transistor #(.\type ("n"), .gate("br")) transistor_20 (
    .in(1'b0), .out(transistor_16_out), .gate(pull_resistor_8_node));
  Pull_Resistor #(.pull(1)) pull_resistor_10 (.node(pull_resistor_10_node));
  Transistor #(.\type ("n"), .gate("br")) transistor_21 (.in(1'b0), .out(pull_resistor_10_node), .gate(data_in__pad));

  assign rd = R_W;
endmodule
