// Logisim project dpmcrevv2.circ as structural Verilog: 15 circuits, main circuit main
module main (
  input  W4010,
  input  W4011,
  input  W4012,
  input  W4013,
  input  W4015,
  input  nR4015,
  input  D0,
  input  D1,
  input  D2,
  input  in_10,
  input  D3,
  input  D4,
  input  in_13,
  input  D5,
  input  D6,
  input  D7,
  input  R_W,
  input  Res,
  output PHI1,
  output PHI2,
  output ACLK,
  output nACLK,
  output D4_2,
  output nDMCINT,
  output D7_2,
  output RUNDMC,
  output out_27,
  output Z4,
  output out_29,
  output out_30,
  output out_31,
  output out_32,
  output out_33,
  output out_34,
  output out_35
);

  wire and_1_out, clock_1_out, controlled_buffer_3_out, dmc_control_1_bload, dmc_control_1_bstep,
       dmc_control_1_dstep, dmc_control_1_nstep, dmc_control_1_pcm, dmc_control_1_sload, dmc_control_1_sstep,
       lfsr_frequency_1_fload, new_dmc_output_counter_1_dout, new_sample_shift_register_1_bout, not_1_out,
       not_2_out, not_3_out, register_1_d0_2, register_1_d1_2, register_1_d2_2, register_1_d3_2,
       register_1_d6_2, register_1_nd7, register_3_d0_2, register_3_d1_2, register_3_d2_2, register_3_d3_2,
       register_3_d4_2, register_3_d5_2, register_3_d6_2, register_3_d7_2, sample_bit_counter_1_nout,
       sample_lenght_counter_1_sout;
  wire [7:0] controlled_buffer_1_out, register_2_d0_2, rom_1_data;
  wire [14:0] address_counter_1_dmc_a0, counter_1_q, register_4_q;
  wire [19:0] counter_3_q;
  wire [23:0] counter_2_q;

  Clock clock_1 (.out(clock_1_out));
  Register register_1 (
    .ACLK(ACLK), .W40xx(W4010), .D0(D0), .D1(D1), .D2(D2), .D3(D3), .D4(D4), .D5(D5), .D6(D6), .D7(D7),
    .D0_2(register_1_d0_2), .D1_2(register_1_d1_2), .D2_2(register_1_d2_2), .D3_2(register_1_d3_2),
    .D6_2(register_1_d6_2), .nD7(register_1_nd7));  // open: D4_2, D5_2, D7_2
  Register register_2 (
    .ACLK(ACLK), .W40xx(W4012), .D0(D0), .D1(D1), .D2(D2), .D3(D3), .D4(D4), .D5(D5), .D6(D6), .D7(D7),
    .D0_2(register_2_d0_2[0]), .D1_2(register_2_d0_2[1]), .D2_2(register_2_d0_2[2]),
    .D3_2(register_2_d0_2[3]), .D4_2(register_2_d0_2[4]), .D5_2(register_2_d0_2[5]),
    .D6_2(register_2_d0_2[6]), .D7_2(register_2_d0_2[7]));  // open: nD7
  Register register_3 (
    .ACLK(ACLK), .W40xx(W4013), .D0(D0), .D1(D1), .D2(D2), .D3(D3), .D4(D4), .D5(D5), .D6(D6), .D7(D7),
    .D0_2(register_3_d0_2), .D1_2(register_3_d1_2), .D2_2(register_3_d2_2), .D3_2(register_3_d3_2),
    .D4_2(register_3_d4_2), .D5_2(register_3_d5_2), .D6_2(register_3_d6_2), .D7_2(register_3_d7_2));  // open: nD7
  Master_clock master_clock_1 (.PHI0(clock_1_out), .RES(Res), .PHI1(PHI1), .PHI2(PHI2), .ACLK(ACLK), .nACLK(nACLK));
  not not_1 (not_1_out, ACLK);
  LFSR_frequency lfsr_frequency_1 (
    .nACLK2(not_1_out), .Res(Res), .F0(register_1_d0_2), .F1(register_1_d1_2), .F2(register_1_d2_2),
    .F3(register_1_d3_2), .FLOAD(lfsr_frequency_1_fload), .nACLK(nACLK));  // open: FSTEP
  Sample_bit_counter sample_bit_counter_1 (
    .nACLK(nACLK), .NSTEP(dmc_control_1_nstep), .RES(Res), .NOUT(sample_bit_counter_1_nout));
  Dmc_control dmc_control_1 (
    .ACLK(ACLK), .nACLK(nACLK), .PHI1(PHI1), .D4(D4), .W4015(W4015), .nR4015(nR4015), .ENIRQ(register_1_nd7),
    .Res(Res), .LOOP(register_1_d6_2), .SOUT(sample_lenght_counter_1_sout), .R_W(R_W),
    .FLOAD(lfsr_frequency_1_fload), .DOUT(new_dmc_output_counter_1_dout), .NOUT(sample_bit_counter_1_nout),
    .D4_2(D4_2), .nDMCINT(nDMCINT), .D7(D7_2), .SSTEP(dmc_control_1_sstep), .SLOAD(dmc_control_1_sload),
    .RUNDMC(RUNDMC), .out_21(out_27), .Z4(Z4), .NSTEP(dmc_control_1_nstep), .DSTEP(dmc_control_1_dstep),
    .PCM(dmc_control_1_pcm), .BLOAD(dmc_control_1_bload), .BSTEP(dmc_control_1_bstep));  // open: nFLOAD
  sample_lenght_counter sample_lenght_counter_1 (
    .nACLK(nACLK), .SLOAD(dmc_control_1_sload), .SSTEP(dmc_control_1_sstep), .RES(Res),
    .LSC0(register_3_d0_2), .LSC1(register_3_d1_2), .LSC2(register_3_d2_2), .LSC3(register_3_d3_2),
    .LSC4(register_3_d4_2), .LSC5(register_3_d5_2), .LSC6(register_3_d6_2), .LSC7(register_3_d7_2),
    .SOUT(sample_lenght_counter_1_sout));
  Address_counter address_counter_1 (
    .nACLK(nACLK), .SLOAD(dmc_control_1_sload), .SSTEP(dmc_control_1_sstep), .RES(Res),
    .LDMC6(register_2_d0_2[0]), .LDMC7(register_2_d0_2[1]), .LDMC8(register_2_d0_2[2]),
    .LDMC9(register_2_d0_2[3]), .LDMC10(register_2_d0_2[4]), .LDMC11(register_2_d0_2[5]),
    .LDMC12(register_2_d0_2[6]), .LDMC13(register_2_d0_2[7]), .DMC_A0(address_counter_1_dmc_a0[0]),
    .DMC_A1(address_counter_1_dmc_a0[1]), .DMC_A2(address_counter_1_dmc_a0[2]),
    .DMC_A3(address_counter_1_dmc_a0[3]), .DMC_A4(address_counter_1_dmc_a0[4]),
    .DMC_A5(address_counter_1_dmc_a0[5]), .DMC_A6(address_counter_1_dmc_a0[6]),
    .DMC_A7(address_counter_1_dmc_a0[7]), .DMC_A8(address_counter_1_dmc_a0[8]),
    .DMC_A9(address_counter_1_dmc_a0[9]), .DMC_A10(address_counter_1_dmc_a0[10]),
    .DMC_A11(address_counter_1_dmc_a0[11]), .DMC_A12(address_counter_1_dmc_a0[12]),
    .DMC_A13(address_counter_1_dmc_a0[13]), .DMC_A14(address_counter_1_dmc_a0[14]));
  assign controlled_buffer_1_out = W4011 ? {D7, D6, D5, D4, D3, D2, D1, D0} : 8'bz;  // Controlled_Buffer controlled_buffer_1
  Counter #(.width(15), .max('h7fff)) counter_1 (
    .Q(counter_1_q), .clk(PHI1), .clr(lfsr_frequency_1_fload));  // open: load, D, count, carry
  Register_part #(.width(15)) register_4 (
    .D(counter_1_q), .Q(register_4_q), .clk(lfsr_frequency_1_fload));  // open: en, clr
  Register_part #(.width(16)) register_5 (
    .D({1'b1, address_counter_1_dmc_a0}), .clk(dmc_control_1_sload));  // open: en, Q, clr
  not not_2 (not_2_out, W4011);
  // Probe on register_4_q
  Counter #(.width(24), .max('hffffff)) counter_2 (
    .Q(counter_2_q), .clk(and_1_out), .clr(in_10));  // open: load, D, count, carry
  and and_1 (and_1_out, lfsr_frequency_1_fload, D4_2);
  // Probe on {1'b1, address_counter_1_dmc_a0}
  assign controlled_buffer_1_out = not_2_out ? rom_1_data : 8'bz;  // Controlled_Buffer controlled_buffer_2
  ROM #(.addrWidth(16)) rom_1 (.addr({1'b1, address_counter_1_dmc_a0}), .data(rom_1_data), .sel(R_W));
  RAM #(.addrWidth(24), .dataWidth(7), .bus("asynch")) ram_1 (
    .addr(counter_2_q), .data({out_35, out_34, out_33, out_32, out_31, out_30, out_29}), .sel(R_W),
    .ld(in_13), .clr(in_10));
  New_dmc_output_counter new_dmc_output_counter_1 (
    .nACLK(nACLK), .ACLK(ACLK), .W4011(W4011), .DSTEP(dmc_control_1_dstep), .RES(Res),
    .BOUT(new_sample_shift_register_1_bout), .DL0(controlled_buffer_1_out[0]),
    .DL1(controlled_buffer_1_out[1]), .DL2(controlled_buffer_1_out[2]), .DL3(controlled_buffer_1_out[3]),
    .DL4(controlled_buffer_1_out[4]), .DL5(controlled_buffer_1_out[5]), .DL6(controlled_buffer_1_out[6]),
    .DMC0(out_29), .DMC1(out_30), .DMC2(out_31), .DMC3(out_32), .DMC4(out_33), .DMC5(out_34), .DMC6(out_35),
    .DOUT(new_dmc_output_counter_1_dout));
  Counter #(.width(20), .max('hfffff)) counter_3 (
    .Q(counter_3_q), .clk(controlled_buffer_3_out), .clr(in_10));  // open: load, D, count, carry
  assign controlled_buffer_3_out = D4_2 ? dmc_control_1_bstep : 1'bz;  // Controlled_Buffer controlled_buffer_3
  New_sample_shift_register new_sample_shift_register_1 (
    .ACLK(1'b0), .nACLK(nACLK), .SL0(controlled_buffer_1_out[0]), .SL1(controlled_buffer_1_out[1]),
    .SL2(controlled_buffer_1_out[2]), .SL3(controlled_buffer_1_out[3]), .SL4(controlled_buffer_1_out[4]),
    .SL5(controlled_buffer_1_out[5]), .SL6(controlled_buffer_1_out[6]), .SL7(controlled_buffer_1_out[7]),
    .BSTEP(dmc_control_1_bstep), .BLOAD(dmc_control_1_bload), .res(Res), .PCM(dmc_control_1_pcm),
    .BOUT(new_sample_shift_register_1_bout));
  not not_3 (not_3_out, 1'b1);
  RAM #(.addrWidth(20), .dataWidth(1), .bus("asynch")) ram_2 (
    .addr(counter_3_q), .data(new_sample_shift_register_1_bout), .sel(1'b1), .ld(not_3_out), .clr(in_10));

  // Notes on the sheet:
  //   C200 test area
  //   sample at c000 lenght 321 bytes
  //   sample at d500 lengh 2500 bytes
  //   sample d200 lenght 17bytes
  //   sample at d300 lenght 369 bytes
  //   sample begin at d100 lengh 177bytes (set dmc output to 64)
  //   contents of rom_1 (hex, n*v repeats v):
  //   49152*0 b5 70 5 ff f0 f ff 0 f0 f b8 5f f0 f0 7f f5 0 f 0 7 84 b0 0 50 7 a8 f f0 ab 5 f ff f5 4f ff
  //   ff 7f ff ff f7 8f 4f f7 f0 a af 48 b 84 0 80 4*0 a b 0 0 a8 40 a0 44 55 55 55 b7 ab f5 ab f7 ab ff
  //   7b ff f5 ff fb bb bf f ff ff 5f ff 78 f7 f0 7a 74 7 57 a4 8a 40 85 40 a 80 50 8 5 a 80 0 0 a 8 a0 a
  //   80 50 4 74 4 b f f ab 5b 75 57 5f f7 57 bf 7f 7b ff f5 7f 7f fa 7b bf 7b af 57 f7 5b fa b5 7a f0 55
  //   55 87 57 a8 5a 48 74 80 ab 0 55 40 7 a5 40 58 a8 40 a 45 a8 50 84 5 55 84 40 45 8a 44 55 a8 85 b4 aa
  //   44 f 4f b5 4a bb 5a 57 af 77 75 bb 75 b7 7b b7 77 af 5f b7 77 b7 5b 5f bb 7a 57 bb 7a 75 f0 b5 54 55
  //   b5 4a 45 85 a5 a8 44 a8 a8 50 88 4a a0 48 44 a8 4 85 a 54 85 44 7 a5 8a 4a 45 47 47 74 74 74 58 75
  //   45 5f f4 f4 78 47 75 f5 ba a5 5f b5 7a 55 77 8f a7 55 57 57 74 bb 8a 5b 75 54 5a a5 aa 5a 4*aa 8a aa
  //   b 55 4b 54 4*55 75 74 70 45 55 55 55 75 45 75 45 55 55 aa 8a 87 aa b4 54 4b 55 55 55 44 55 55 55 5a
  //   f0 191*0 ff 0 ff 0 ff 0 ff 0 ff 0 ff 0 ff 0 ff 0 0 ff 0 ff 0 ff 0 ff 0 ff 0 ff 0 ff 0 ff 16*55
  //   3792*0 5*aa af f0 9e 9f f0 6 ae 7c 1b 98 f0 0 3 0 c 1 ce 1 80 5*0 f 1f ff fb f3 cf f3 ef de b8 f9 a6
  //   a2 24 39 81 43 80 86 19 2 38 51 87 86 15 39 8c a6 55 4d 16 8c a3 45 45 90 ca 56 22 52 70 d6 53 16 d3
  //   54 d7 4b 37 4b 5b 6b 56 ce b5 5b 5d 59 b6 d5 ab d6 b5 d7 6b 6d ad ae b6 d6 b5 b5 aa d6 aa ac aa a9
  //   54 a9 94 a4 a9 4a 4a 8a 92 54 a5 49 29 4a 54 a5 29 52 a5 4a a5 54 a9 54 aa 95 2a aa 94 95 2a aa 55
  //   55 2a 56 66 aa 9a aa b5 5a ad ab 5a b5 6b 6b 6b 5a b5 aa b5 56 aa d5 55 56 7*aa 95 55 55 ff 79*0 3f
  //   fc 7f dc e1 f9 f df f7 0 0 0 80 fd ff ff ff 239*0 fe ff de ff e3 ef 8c 44 40 31 37 9 80 18 60 0 c0
  //   20 2f 3a a3 57 ef 9f af ff de bf 9e c9 24 41 9 0 4 0 18 74 9b bf 76 eb cf 7b df f3 81 e2 68 31 1c 31
  //   88 6a c0 8f 6 d4 c5 c7 2f 1d 63 a7 d0 fc 63 cf b8 dc 76 33 ee 30 e2 d0 8 38 84 1 42 1e 7d 9e 7f e7
  //   ef 3f 7f 3f 87 dc 63 18 88 53 11 6 d 62 3 3c 33 24 e7 1f f8 f0 f3 cf 71 ae 1c 8e cf 8 ce c2 40 e1 8e
  //   18 2c d1 91 ed 9f f cf c7 cc f5 38 39 b8 19 47 88 46 d6 4 58 63 9c 61 79 8c f3 98 f7 78 27 c7 f 8c
  //   f5 86 2f 91 8c 71 c7 21 e1 c4 7 a6 2e 8a e7 43 cf 9e 1f 9e 71 f3 63 c3 18 c3 b0 e0 e3 f 8 e0 71 8c
  //   39 39 99 f1 bc 74 76 e2 f3 c7 97 19 c6 37 f 9 c6 71 23 88 e0 a9 83 8b 8c ef d da f4 73 ee 1c db 8e
  //   76 1a 2e 31 c3 9c 59 7 a1 c0 f1 19 9c 58 3c e3 39 e3 8e b8 e7 1c e3 a7 d 8e c2 39 e6 26 36 19 8c 74
  //   98 cd 47 38 b8 f2 6e ac b3 b4 e5 71 27 8e 8c 8f 8e 1c 6b 29 8e 1c 2c 68 d9 31 e3 55 97 38 d3 b1 ce
  //   38 f1 d4 b3 4e a9 62 c9 a8 ac a9 18 e6 51 9a 73 29 9e 39 d3 65 9d 58 ba 61 da 46 aa 3c 52 b1 31 e0
  //   e5 95 2a cc b2 9c ac ab 39 66 6a cc ab 8b 55 a6 a6 aa 3c 5a 39 38 b9 54 aa 95 aa 65 5a 9c c7 59 b2
  //   ae d4 b1 d4 63 c5 34 6a 65 69 65 4c e3 143*0 1 0 ad aa ea ff bf e9 f 80 f f8 7f 0 fe f c0 cf 40 7b
  //   80 3f 80 9f 82 ff a4 81 ff 0 f0 7f e0 ef f 80 cf 1b 0 f9 6f 50 e0 ff 0 f 12 fc fe d c0 81 7b 8c fb 1
  //   fe 1 f8 7 0 fe ff aa aa 54 5*55 15 c0 ff 31 c0 ff 0 f8 3 f0 3f f8 1f 0 ff 3 80 f7 3 3f f0 80 ff c1 f
  //   38 c0 9f f4 9e f8 0 7c fc b0 5f f8 1f 48 c0 e 88 7 fc ef 1 fe 3f fe f7 1 4*0 fe ff c0 ff ff 3f 55 55
  //   55 a5 4*aa f4 4*0 e0 4*ff 7f 0 0 0 7 0 fe ff c8 ff ff 7f 0 0 60 2 0 fe ff ff ff 1f 0 0 0 4f 0 fe ff
  //   ff ff 1f 0 0 a0 0 c0 4*ff 7 0 0 1b 0 e0 4*ff 5f aa 2a 55 55 aa aa 54 55 1 0 0 6 a0 d0 ff fd ff 1f 0
  //   0 f0 7 7c 0 fe ff ff 0 0 dc f f0 7 0 ff ff 1f 0 70 f0 c7 1f 0 f0 ff ff 1 0 6a ff 78 0 80 ff ff 1f 0
  //   1c fc eb 7 0 f0 ff ff 0 40 f0 7f 7*55 f5 e1 7 0 f0 ff ff 1 0 c0 ff ff 0 0 fc ff 1f 0 0 fa ff f 0 e0
  //   ff ff 0 40 c0 ff ff 0 0 ff ff 3 0 2 fe ff f 0 f8 ff 1f 0 0 f8 ff 7f 0 c0 ff ff 0 0 82 ff ff 1 0 0 80
  //   aa 5a 55 d5 aa aa f6 ff ff f 80 f ff ff 3 0 fc ff f 0 60 f8 ff 1f 0 80 ff ff 0 0 af fe 7f 0 0 fe ff
  //   3 0 78 fb ff 1 0 f0 ff 7f 0 0 ff ef b 0 c0 ff ff 3 0 ec fd b6 0 0 fc ff f 0 0 0 b5 aa aa 5a 55 55 85
  //   ff ff ff 7 0 f8 ff 7f 0 80 ff af 4c 0 80 ff ff 7 0 ec fd cd 1 0 fc ff f 0 dc bf 40 17 0 f0 ff ff 1 0
  //   ff 47 72 0 80 ff ff f 0 f8 7f c0 5 0 fe ff 7f 0 80 ff 3 5c 4*55 4*aa 2a 1 74 ff ff f 0 e0 ff 0 3 40
  //   ff ff bf 0 80 ff 3 a c0 f5 ff ff 1 0 f8 27 29 2 da fe ff 1f 0 c0 3b 62 4 a9 ff ff 3f 0 80 2e ca 24
  //   74 b7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
endmodule

module Table (
  input  F3,
  input  F2,
  input  F1,
  input  F0,
  output LP0,
  output LP1,
  output LP2,
  output LP3,
  output LP4,
  output LP5,
  output LP6,
  output LP7,
  output LP8
);

  wire not_1_out, not_2_out, not_3_out, not_4_out, transistor_9_out, transistor_18_out, transistor_19_out,
       transistor_31_out, transistor_42_out, transistor_50_out, transistor_51_out, transistor_65_out,
       transistor_73_out, transistor_83_out, transistor_89_out, transistor_90_out, transistor_100_out,
       transistor_115_out, transistor_122_out, transistor_123_out;

  not not_1 (not_1_out, F3);
  not not_2 (not_2_out, F2);
  not not_3 (not_3_out, F1);
  not not_4 (not_4_out, F0);
  Transistor #(.\type ("n"), .gate("br")) transistor_1 (.in(1'b0), .out(LP1), .gate(transistor_9_out));
  Transistor #(.\type ("n"), .gate("br")) transistor_2 (.in(1'b0), .out(LP2), .gate(transistor_18_out));
  Transistor #(.\type ("n"), .gate("br")) transistor_3 (.in(1'b0), .out(LP3), .gate(transistor_9_out));
  Transistor #(.\type ("n"), .gate("br")) transistor_4 (.in(1'b0), .out(LP3), .gate(transistor_18_out));
  Transistor #(.\type ("n"), .gate("br")) transistor_5 (.in(1'b0), .out(LP4), .gate(transistor_18_out));
  Transistor #(.\type ("n"), .gate("br")) transistor_6 (.in(1'b0), .out(LP5), .gate(transistor_9_out));
  Transistor #(.\type ("n"), .gate("br")) transistor_7 (.in(1'b0), .out(LP8), .gate(transistor_18_out));
  Transistor #(.\type ("n"), .gate("br")) transistor_8 (.in(1'b0), .out(LP8), .gate(transistor_9_out));
  Transistor #(.\type ("n")) transistor_9 (.in(1'b0), .out(transistor_9_out), .gate(not_1_out));
  Transistor #(.\type ("n")) transistor_10 (.in(1'b0), .out(transistor_9_out), .gate(not_2_out));
  Transistor #(.\type ("n")) transistor_11 (.in(1'b0), .out(transistor_9_out), .gate(not_3_out));
  Transistor #(.\type ("n")) transistor_12 (.in(1'b0), .out(transistor_9_out), .gate(not_4_out));
  Pull_Resistor #(.pull(1)) pull_resistor_1 (.node(transistor_9_out));
  Transistor #(.\type ("n"), .gate("br")) transistor_13 (.in(1'b0), .out(LP2), .gate(transistor_19_out));
  Transistor #(.\type ("n"), .gate("br")) transistor_14 (.in(1'b0), .out(LP3), .gate(transistor_19_out));
  Transistor #(.\type ("n"), .gate("br")) transistor_15 (.in(1'b0), .out(LP4), .gate(transistor_19_out));
  Transistor #(.\type ("n"), .gate("br")) transistor_16 (.in(1'b0), .out(LP6), .gate(transistor_19_out));
  Transistor #(.\type ("n"), .gate("br")) transistor_17 (.in(1'b0), .out(LP7), .gate(transistor_19_out));
  Transistor #(.\type ("n")) transistor_18 (.in(1'b0), .out(transistor_18_out), .gate(not_1_out));
  Transistor #(.\type ("n")) transistor_19 (.in(1'b0), .out(transistor_19_out), .gate(not_1_out));
  Transistor #(.\type ("n")) transistor_20 (.in(1'b0), .out(transistor_18_out), .gate(not_2_out));
  Transistor #(.\type ("n")) transistor_21 (.in(1'b0), .out(transistor_19_out), .gate(not_2_out));
  Transistor #(.\type ("n")) transistor_22 (.in(1'b0), .out(transistor_19_out), .gate(F1));
  Transistor #(.\type ("n")) transistor_23 (.in(1'b0), .out(transistor_18_out), .gate(not_3_out));
  Transistor #(.\type ("n")) transistor_24 (.in(1'b0), .out(transistor_18_out), .gate(F0));
  Transistor #(.\type ("n")) transistor_25 (.in(1'b0), .out(transistor_19_out), .gate(not_4_out));
  Pull_Resistor #(.pull(1)) pull_resistor_2 (.node(transistor_19_out));
  Pull_Resistor #(.pull(1)) pull_resistor_3 (.node(transistor_18_out));
  Transistor #(.\type ("n"), .gate("br")) transistor_26 (.in(1'b0), .out(LP0), .gate(transistor_31_out));
  Transistor #(.\type ("n"), .gate("br")) transistor_27 (.in(1'b0), .out(LP2), .gate(transistor_31_out));
  Transistor #(.\type ("n"), .gate("br")) transistor_28 (.in(1'b0), .out(LP3), .gate(transistor_31_out));
  Transistor #(.\type ("n"), .gate("br")) transistor_29 (.in(1'b0), .out(LP4), .gate(transistor_31_out));
  Transistor #(.\type ("n"), .gate("br")) transistor_30 (.in(1'b0), .out(LP7), .gate(transistor_31_out));
  Transistor #(.\type ("n")) transistor_31 (.in(1'b0), .out(transistor_31_out), .gate(not_1_out));
  Transistor #(.\type ("n")) transistor_32 (.in(1'b0), .out(transistor_31_out), .gate(not_2_out));
  Transistor #(.\type ("n")) transistor_33 (.in(1'b0), .out(transistor_31_out), .gate(F1));
  Transistor #(.\type ("n")) transistor_34 (.in(1'b0), .out(transistor_31_out), .gate(F0));
  Pull_Resistor #(.pull(1)) pull_resistor_4 (.node(transistor_31_out));
  Transistor #(.\type ("n"), .gate("br")) transistor_35 (.in(1'b0), .out(LP0), .gate(transistor_42_out));
  Transistor #(.\type ("n"), .gate("br")) transistor_36 (.in(1'b0), .out(LP0), .gate(transistor_51_out));
  Transistor #(.\type ("n"), .gate("br")) transistor_37 (.in(1'b0), .out(LP5), .gate(transistor_51_out));
  Transistor #(.\type ("n"), .gate("br")) transistor_38 (.in(1'b0), .out(LP6), .gate(transistor_51_out));
  Transistor #(.\type ("n"), .gate("br")) transistor_39 (.in(1'b0), .out(LP6), .gate(transistor_42_out));
  Transistor #(.\type ("n"), .gate("br")) transistor_40 (.in(1'b0), .out(LP7), .gate(transistor_51_out));
  Transistor #(.\type ("n"), .gate("br")) transistor_41 (.in(1'b0), .out(LP7), .gate(transistor_42_out));
  Transistor #(.\type ("n")) transistor_42 (.in(1'b0), .out(transistor_42_out), .gate(not_1_out));
  Transistor #(.\type ("n")) transistor_43 (.in(1'b0), .out(transistor_42_out), .gate(F2));
  Transistor #(.\type ("n")) transistor_44 (.in(1'b0), .out(transistor_42_out), .gate(not_3_out));
  Transistor #(.\type ("n")) transistor_45 (.in(1'b0), .out(transistor_42_out), .gate(not_4_out));
  Pull_Resistor #(.pull(1)) pull_resistor_5 (.node(transistor_42_out));
  Transistor #(.\type ("n"), .gate("br")) transistor_46 (.in(1'b0), .out(LP0), .gate(transistor_50_out));
  Transistor #(.\type ("n"), .gate("br")) transistor_47 (.in(1'b0), .out(LP3), .gate(transistor_50_out));
  Transistor #(.\type ("n"), .gate("br")) transistor_48 (.in(1'b0), .out(LP7), .gate(transistor_50_out));
  Transistor #(.\type ("n"), .gate("br")) transistor_49 (.in(1'b0), .out(LP8), .gate(transistor_50_out));
  Transistor #(.\type ("n")) transistor_50 (.in(1'b0), .out(transistor_50_out), .gate(not_1_out));
  Transistor #(.\type ("n")) transistor_51 (.in(1'b0), .out(transistor_51_out), .gate(not_1_out));
  Transistor #(.\type ("n")) transistor_52 (.in(1'b0), .out(transistor_51_out), .gate(F2));
  Transistor #(.\type ("n")) transistor_53 (.in(1'b0), .out(transistor_50_out), .gate(F2));
  Transistor #(.\type ("n")) transistor_54 (.in(1'b0), .out(transistor_50_out), .gate(F1));
  Transistor #(.\type ("n")) transistor_55 (.in(1'b0), .out(transistor_51_out), .gate(not_3_out));
  Transistor #(.\type ("n")) transistor_56 (.in(1'b0), .out(transistor_51_out), .gate(F0));
  Transistor #(.\type ("n")) transistor_57 (.in(1'b0), .out(transistor_50_out), .gate(not_4_out));
  Pull_Resistor #(.pull(1)) pull_resistor_6 (.node(transistor_50_out));
  Pull_Resistor #(.pull(1)) pull_resistor_7 (.node(transistor_51_out));
  Transistor #(.\type ("n"), .gate("br")) transistor_58 (.in(1'b0), .out(LP0), .gate(transistor_65_out));
  Transistor #(.\type ("n"), .gate("br")) transistor_59 (.in(1'b0), .out(LP1), .gate(transistor_65_out));
  Transistor #(.\type ("n"), .gate("br")) transistor_60 (.in(1'b0), .out(LP2), .gate(transistor_65_out));
  Transistor #(.\type ("n"), .gate("br")) transistor_61 (.in(1'b0), .out(LP3), .gate(transistor_65_out));
  Transistor #(.\type ("n"), .gate("br")) transistor_62 (.in(1'b0), .out(LP4), .gate(transistor_65_out));
  Transistor #(.\type ("n"), .gate("br")) transistor_63 (.in(1'b0), .out(LP6), .gate(transistor_65_out));
  Transistor #(.\type ("n"), .gate("br")) transistor_64 (.in(1'b0), .out(LP7), .gate(transistor_65_out));
  Transistor #(.\type ("n")) transistor_65 (.in(1'b0), .out(transistor_65_out), .gate(not_1_out));
  Transistor #(.\type ("n")) transistor_66 (.in(1'b0), .out(transistor_65_out), .gate(F2));
  Transistor #(.\type ("n")) transistor_67 (.in(1'b0), .out(transistor_65_out), .gate(F1));
  Transistor #(.\type ("n")) transistor_68 (.in(1'b0), .out(transistor_65_out), .gate(F0));
  Pull_Resistor #(.pull(1)) pull_resistor_8 (.node(transistor_65_out));
  Transistor #(.\type ("n"), .gate("br")) transistor_69 (.in(1'b0), .out(LP3), .gate(transistor_73_out));
  Transistor #(.\type ("n"), .gate("br")) transistor_70 (.in(1'b0), .out(LP5), .gate(transistor_73_out));
  Transistor #(.\type ("n"), .gate("br")) transistor_71 (.in(1'b0), .out(LP6), .gate(transistor_73_out));
  Transistor #(.\type ("n"), .gate("br")) transistor_72 (.in(1'b0), .out(LP7), .gate(transistor_73_out));
  Transistor #(.\type ("n")) transistor_73 (.in(1'b0), .out(transistor_73_out), .gate(F3));
  Transistor #(.\type ("n")) transistor_74 (.in(1'b0), .out(transistor_73_out), .gate(not_2_out));
  Transistor #(.\type ("n")) transistor_75 (.in(1'b0), .out(transistor_73_out), .gate(not_3_out));
  Transistor #(.\type ("n")) transistor_76 (.in(1'b0), .out(transistor_73_out), .gate(not_4_out));
  Pull_Resistor #(.pull(1)) pull_resistor_9 (.node(transistor_73_out));
  Transistor #(.\type ("n"), .gate("br")) transistor_77 (.in(1'b0), .out(LP0), .gate(transistor_83_out));
  Transistor #(.\type ("n"), .gate("br")) transistor_78 (.in(1'b0), .out(LP0), .gate(transistor_90_out));
  Transistor #(.\type ("n"), .gate("br")) transistor_79 (.in(1'b0), .out(LP1), .gate(transistor_90_out));
  Transistor #(.\type ("n"), .gate("br")) transistor_80 (.in(1'b0), .out(LP1), .gate(transistor_83_out));
  Transistor #(.\type ("n"), .gate("br")) transistor_81 (.in(1'b0), .out(LP2), .gate(transistor_90_out));
  Transistor #(.\type ("n"), .gate("br")) transistor_82 (.in(1'b0), .out(LP7), .gate(transistor_83_out));
  Transistor #(.\type ("n")) transistor_83 (.in(1'b0), .out(transistor_83_out), .gate(F3));
  Transistor #(.\type ("n")) transistor_84 (.in(1'b0), .out(transistor_83_out), .gate(not_2_out));
  Transistor #(.\type ("n")) transistor_85 (.in(1'b0), .out(transistor_83_out), .gate(not_3_out));
  Transistor #(.\type ("n")) transistor_86 (.in(1'b0), .out(transistor_83_out), .gate(F0));
  Pull_Resistor #(.pull(1)) pull_resistor_10 (.node(transistor_83_out));
  Transistor #(.\type ("n"), .gate("br")) transistor_87 (.in(1'b0), .out(LP4), .gate(transistor_89_out));
  Transistor #(.\type ("n"), .gate("br")) transistor_88 (.in(1'b0), .out(LP8), .gate(transistor_89_out));
  Transistor #(.\type ("n")) transistor_89 (.in(1'b0), .out(transistor_89_out), .gate(F3));
  Transistor #(.\type ("n")) transistor_90 (.in(1'b0), .out(transistor_90_out), .gate(F3));
  Transistor #(.\type ("n")) transistor_91 (.in(1'b0), .out(transistor_89_out), .gate(not_2_out));
  Transistor #(.\type ("n")) transistor_92 (.in(1'b0), .out(transistor_90_out), .gate(not_2_out));
  Transistor #(.\type ("n")) transistor_93 (.in(1'b0), .out(transistor_90_out), .gate(F1));
  Transistor #(.\type ("n")) transistor_94 (.in(1'b0), .out(transistor_89_out), .gate(F1));
  Transistor #(.\type ("n")) transistor_95 (.in(1'b0), .out(transistor_89_out), .gate(F0));
  Transistor #(.\type ("n")) transistor_96 (.in(1'b0), .out(transistor_90_out), .gate(not_4_out));
  Pull_Resistor #(.pull(1)) pull_resistor_11 (.node(transistor_89_out));
  Pull_Resistor #(.pull(1)) pull_resistor_12 (.node(transistor_90_out));
  Transistor #(.\type ("n"), .gate("br")) transistor_97 (.in(1'b0), .out(LP0), .gate(transistor_100_out));
  Transistor #(.\type ("n"), .gate("br")) transistor_98 (.in(1'b0), .out(LP3), .gate(transistor_100_out));
  Transistor #(.\type ("n"), .gate("br")) transistor_99 (.in(1'b0), .out(LP6), .gate(transistor_100_out));
  Transistor #(.\type ("n")) transistor_100 (.in(1'b0), .out(transistor_100_out), .gate(F3));
  Transistor #(.\type ("n")) transistor_101 (.in(1'b0), .out(transistor_100_out), .gate(F2));
  Transistor #(.\type ("n")) transistor_102 (.in(1'b0), .out(transistor_100_out), .gate(not_3_out));
  Transistor #(.\type ("n")) transistor_103 (.in(1'b0), .out(transistor_100_out), .gate(not_4_out));
  Pull_Resistor #(.pull(1)) pull_resistor_13 (.node(transistor_100_out));
  Transistor #(.\type ("n"), .gate("br")) transistor_104 (.in(1'b0), .out(LP0), .gate(transistor_123_out));
  Transistor #(.\type ("n"), .gate("br")) transistor_105 (.in(1'b0), .out(LP1), .gate(transistor_115_out));
  Transistor #(.\type ("n"), .gate("br")) transistor_106 (.in(1'b0), .out(LP2), .gate(transistor_123_out));
  Transistor #(.\type ("n"), .gate("br")) transistor_107 (.in(1'b0), .out(LP3), .gate(transistor_115_out));
  Transistor #(.\type ("n"), .gate("br")) transistor_108 (.in(1'b0), .out(LP3), .gate(transistor_123_out));
  Transistor #(.\type ("n"), .gate("br")) transistor_109 (.in(1'b0), .out(LP4), .gate(transistor_115_out));
  Transistor #(.\type ("n"), .gate("br")) transistor_110 (.in(1'b0), .out(LP4), .gate(transistor_123_out));
  Transistor #(.\type ("n"), .gate("br")) transistor_111 (.in(1'b0), .out(LP5), .gate(transistor_115_out));
  Transistor #(.\type ("n"), .gate("br")) transistor_112 (.in(1'b0), .out(LP6), .gate(transistor_115_out));
  Transistor #(.\type ("n"), .gate("br")) transistor_113 (.in(1'b0), .out(LP6), .gate(transistor_123_out));
  Transistor #(.\type ("n"), .gate("br")) transistor_114 (.in(1'b0), .out(LP8), .gate(transistor_123_out));
  Transistor #(.\type ("n")) transistor_115 (.in(1'b0), .out(transistor_115_out), .gate(F3));
  Transistor #(.\type ("n")) transistor_116 (.in(1'b0), .out(transistor_115_out), .gate(F2));
  Transistor #(.\type ("n")) transistor_117 (.in(1'b0), .out(transistor_115_out), .gate(not_3_out));
  Transistor #(.\type ("n")) transistor_118 (.in(1'b0), .out(transistor_115_out), .gate(F0));
  Pull_Resistor #(.pull(1)) pull_resistor_14 (.node(transistor_115_out));
  Transistor #(.\type ("n"), .gate("br")) transistor_119 (.in(1'b0), .out(LP1), .gate(transistor_122_out));
  Transistor #(.\type ("n"), .gate("br")) transistor_120 (.in(1'b0), .out(LP5), .gate(transistor_122_out));
  Transistor #(.\type ("n"), .gate("br")) transistor_121 (.in(1'b0), .out(LP6), .gate(transistor_122_out));
  Transistor #(.\type ("n")) transistor_122 (.in(1'b0), .out(transistor_122_out), .gate(F3));
  Transistor #(.\type ("n")) transistor_123 (.in(1'b0), .out(transistor_123_out), .gate(F3));
  Transistor #(.\type ("n")) transistor_124 (.in(1'b0), .out(transistor_122_out), .gate(F2));
  Transistor #(.\type ("n")) transistor_125 (.in(1'b0), .out(transistor_123_out), .gate(F2));
  Transistor #(.\type ("n")) transistor_126 (.in(1'b0), .out(transistor_123_out), .gate(F1));
  Transistor #(.\type ("n")) transistor_127 (.in(1'b0), .out(transistor_122_out), .gate(F1));
  Transistor #(.\type ("n")) transistor_128 (.in(1'b0), .out(transistor_122_out), .gate(F0));
  Transistor #(.\type ("n")) transistor_129 (.in(1'b0), .out(transistor_123_out), .gate(not_4_out));
  Pull_Resistor #(.pull(1)) pull_resistor_15 (.node(transistor_122_out));
  Pull_Resistor #(.pull(1)) pull_resistor_16 (.node(transistor_123_out));
  Pull_Resistor #(.pull(1)) pull_resistor_17 (.node(LP0));
  Pull_Resistor #(.pull(1)) pull_resistor_18 (.node(LP1));
  Pull_Resistor #(.pull(1)) pull_resistor_19 (.node(LP2));
  Pull_Resistor #(.pull(1)) pull_resistor_20 (.node(LP3));
  Pull_Resistor #(.pull(1)) pull_resistor_21 (.node(LP4));
  Pull_Resistor #(.pull(1)) pull_resistor_22 (.node(LP5));
  Pull_Resistor #(.pull(1)) pull_resistor_23 (.node(LP6));
  Pull_Resistor #(.pull(1)) pull_resistor_24 (.node(LP7));
  Pull_Resistor #(.pull(1)) pull_resistor_25 (.node(LP8));
endmodule

module Dlatch (
  input  EN,
  input  IN,
  output Q,
  output nQ
);

  D_Flip_Flop #(.trigger("high")) d_ff_1 (.clk(EN), .D(IN), .Q(Q), .Qn(nQ));  // open: preset, en, reset
endmodule

module Dpos (
  input  Clk,
  input  In,
  output Q,
  output nQ
);

  D_Flip_Flop d_ff_1 (.clk(Clk), .D(In), .Q(Q), .Qn(nQ));  // open: preset, en, reset
endmodule

module LFSR_frequency (
  input  nACLK,
  input  nACLK2,
  input  Res,
  input  F0,
  input  F1,
  input  F2,
  input  F3,
  output FSTEP,
  output FLOAD
);

  wire and_1_out, and_2_out, and_3_out, and_4_out, and_5_out, and_6_out, and_7_out, and_8_out, and_9_out,
       and_10_out, and_11_out, and_12_out, and_13_out, and_14_out, and_15_out, and_16_out, and_17_out,
       and_18_out, and_19_out, d_ff_1_qn, d_ff_2_qn, d_ff_3_qn, d_ff_4_qn, d_ff_5_qn, d_ff_6_qn, d_ff_7_qn,
       d_ff_8_qn, d_ff_9_qn, d_ff_10_qn, d_ff_11_qn, d_ff_12_qn, d_ff_13_qn, d_ff_14_qn, d_ff_15_qn,
       d_ff_16_qn, d_ff_17_qn, d_ff_18_qn, nor_3_out, nor_4_out, nor_5_out, nor_6_out, nor_7_out, not_1_out,
       not_2_out, not_3_out, not_4_out, not_5_out, not_6_out, not_7_out, not_8_out, not_9_out, not_10_out,
       not_11_out, not_12_out, not_13_out, table_1_lp0, table_1_lp1, table_1_lp2, table_1_lp3, table_1_lp4,
       table_1_lp5, table_1_lp6, table_1_lp7, table_1_lp8;

  Table table_1 (
    .LP0(table_1_lp0), .LP1(table_1_lp1), .LP2(table_1_lp2), .LP3(table_1_lp3), .LP4(table_1_lp4),
    .LP5(table_1_lp5), .LP6(table_1_lp6), .LP7(table_1_lp7), .LP8(table_1_lp8), .F3(F3), .F2(F2), .F1(F1),
    .F0(F0));
  not not_1 (not_1_out, nACLK2);
  nor nor_1 (FSTEP, not_1_out, nor_7_out);
  nor nor_2 (FLOAD, not_1_out, not_11_out);
  and and_1 (and_1_out, d_ff_14_qn, d_ff_18_qn);
  nor nor_3 (nor_3_out, nor_5_out, d_ff_14_qn, d_ff_18_qn);
  nor nor_4 (nor_4_out, nor_3_out, Res, and_1_out);
  and and_2 (and_2_out, FLOAD, table_1_lp0);
  and and_3 (and_3_out, FLOAD, not_2_out);
  not not_2 (not_2_out, table_1_lp0);
  and and_4 (and_4_out, FLOAD, table_1_lp1);
  and and_5 (and_5_out, FLOAD, not_3_out);
  not not_3 (not_3_out, table_1_lp1);
  and and_6 (and_6_out, FLOAD, table_1_lp2);
  and and_7 (and_7_out, FLOAD, not_4_out);
  not not_4 (not_4_out, table_1_lp2);
  and and_8 (and_8_out, FLOAD, table_1_lp3);
  and and_9 (and_9_out, FLOAD, not_5_out);
  not not_5 (not_5_out, table_1_lp3);
  and and_10 (and_10_out, FLOAD, table_1_lp4);
  and and_11 (and_11_out, FLOAD, not_6_out);
  not not_6 (not_6_out, table_1_lp4);
  and and_12 (and_12_out, FLOAD, table_1_lp5);
  and and_13 (and_13_out, FLOAD, not_7_out);
  not not_7 (not_7_out, table_1_lp5);
  and and_14 (and_14_out, FLOAD, table_1_lp6);
  and and_15 (and_15_out, FLOAD, not_8_out);
  not not_8 (not_8_out, table_1_lp6);
  and and_16 (and_16_out, FLOAD, table_1_lp7);
  and and_17 (and_17_out, FLOAD, not_9_out);
  not not_9 (not_9_out, table_1_lp7);
  and and_18 (and_18_out, FLOAD, table_1_lp8);
  and and_19 (and_19_out, FLOAD, not_10_out);
  not not_10 (not_10_out, table_1_lp8);
  not not_11 (not_11_out, nor_7_out);
  D_Flip_Flop d_ff_1 (
    .clk(FSTEP), .D(nor_4_out), .Qn(d_ff_1_qn), .preset(and_2_out), .reset(and_3_out));  // open: Q, en
  D_Flip_Flop d_ff_2 (
    .clk(FSTEP), .D(d_ff_10_qn), .Qn(d_ff_2_qn), .preset(and_4_out), .reset(and_5_out));  // open: Q, en
  D_Flip_Flop d_ff_3 (
    .clk(FSTEP), .D(d_ff_11_qn), .Qn(d_ff_3_qn), .preset(and_6_out), .reset(and_7_out));  // open: Q, en
  D_Flip_Flop d_ff_4 (
    .clk(FSTEP), .D(d_ff_12_qn), .Qn(d_ff_4_qn), .preset(and_8_out), .reset(and_9_out));  // open: Q, en
  D_Flip_Flop d_ff_5 (
    .clk(FSTEP), .D(d_ff_13_qn), .Qn(d_ff_5_qn), .preset(and_10_out), .reset(and_11_out));  // open: Q, en
  D_Flip_Flop d_ff_6 (
    .clk(FSTEP), .D(d_ff_14_qn), .Qn(d_ff_6_qn), .preset(and_12_out), .reset(and_13_out));  // open: Q, en
  D_Flip_Flop d_ff_7 (
    .clk(FSTEP), .D(d_ff_15_qn), .Qn(d_ff_7_qn), .preset(and_14_out), .reset(and_15_out));  // open: Q, en
  D_Flip_Flop d_ff_8 (
    .clk(FSTEP), .D(d_ff_16_qn), .Qn(d_ff_8_qn), .preset(and_16_out), .reset(and_17_out));  // open: Q, en
  D_Flip_Flop d_ff_9 (
    .clk(FSTEP), .D(d_ff_17_qn), .Qn(d_ff_9_qn), .preset(and_18_out), .reset(and_19_out));  // open: Q, en
  D_Flip_Flop d_ff_10 (.clk(nACLK), .D(d_ff_1_qn), .Qn(d_ff_10_qn));  // open: Q, preset, en, reset
  D_Flip_Flop d_ff_11 (.clk(nACLK), .D(d_ff_2_qn), .Qn(d_ff_11_qn));  // open: Q, preset, en, reset
  D_Flip_Flop d_ff_12 (.clk(nACLK), .D(d_ff_3_qn), .Qn(d_ff_12_qn));  // open: Q, preset, en, reset
  D_Flip_Flop d_ff_13 (.clk(nACLK), .D(d_ff_4_qn), .Qn(d_ff_13_qn));  // open: Q, preset, en, reset
  D_Flip_Flop d_ff_14 (.clk(nACLK), .D(d_ff_5_qn), .Qn(d_ff_14_qn));  // open: Q, preset, en, reset
  D_Flip_Flop d_ff_15 (.clk(nACLK), .D(d_ff_6_qn), .Qn(d_ff_15_qn));  // open: Q, preset, en, reset
  D_Flip_Flop d_ff_16 (.clk(nACLK), .D(d_ff_7_qn), .Qn(d_ff_16_qn));  // open: Q, preset, en, reset
  D_Flip_Flop d_ff_17 (.clk(nACLK), .D(d_ff_8_qn), .Qn(d_ff_17_qn));  // open: Q, preset, en, reset
  D_Flip_Flop d_ff_18 (.clk(nACLK), .D(d_ff_9_qn), .Qn(d_ff_18_qn));  // open: Q, preset, en, reset
  nor nor_5 (nor_5_out, d_ff_10_qn, d_ff_11_qn, d_ff_12_qn, d_ff_13_qn, d_ff_14_qn, d_ff_15_qn, d_ff_16_qn, d_ff_17_qn, d_ff_18_qn);
  nor nor_6 (nor_6_out, d_ff_10_qn, d_ff_11_qn, d_ff_12_qn, d_ff_13_qn, d_ff_14_qn, d_ff_15_qn, d_ff_16_qn, d_ff_17_qn, not_12_out);
  not not_12 (not_12_out, d_ff_18_qn);
  nor nor_7 (nor_7_out, not_13_out, Res);
  not not_13 (not_13_out, nor_6_out);

  // Notes on the sheet:
  //   NOR1
  //   NOR2
  //   NOR3
  //   INV3
endmodule

module Dmc_control (
  input  ACLK,
  input  nACLK,
  input  PHI1,
  input  D4,
  input  W4015,
  input  nR4015,
  input  ENIRQ,
  input  Res,
  input  LOOP,
  input  SOUT,
  input  R_W,
  input  FLOAD,
  input  DOUT,
  input  NOUT,
  output D4_2,
  output nDMCINT,
  output D7,
  output SSTEP,
  output SLOAD,
  output RUNDMC,
  output out_21,
  output Z4,
  output NSTEP,
  output nFLOAD,
  output DSTEP,
  output PCM,
  output BLOAD,
  output BSTEP
);

  wire and_1_out, and_2_out, and_3_out, d_ff_1_q, d_ff_2_q, d_ff_3_qn, d_ff_4_qn, d_ff_5_q, d_ff_5_qn,
       d_ff_6_q, d_ff_7_qn, d_ff_8_q, d_ff_9_q, d_ff_10_qn, d_ff_11_q, d_ff_12_qn, d_ff_13_q, d_ff_15_qn,
       nand_1_out, nor_1_out, nor_3_out, nor_5_out, nor_7_out, nor_8_out, nor_11_out, not_2_out, not_3_out,
       not_4_out, not_5_out, not_6_out, not_7_out, not_8_out, not_10_out, or_1_out, or_2_out, or_3_out,
       or_4_out, or_5_out, or_6_out, s_r_ff_1_q, s_r_ff_2_qn, s_r_ff_3_qn, s_r_ff_4_qn, s_r_ff_5_q,
       s_r_ff_6_q, s_r_ff_6_qn;
  wire [7:0] counter_2_q;

  not not_1 (nFLOAD, FLOAD);
  D_Flip_Flop d_ff_1 (.clk(nACLK), .D(DOUT), .Q(d_ff_1_q));  // open: Qn, preset, en, reset
  D_Flip_Flop d_ff_2 (.clk(nACLK), .D(s_r_ff_1_q), .Q(d_ff_2_q));  // open: Qn, preset, en, reset
  or or_1 (or_1_out, nor_1_out, Res);
  nor nor_1 (nor_1_out, nFLOAD, not_2_out, NOUT);
  not not_2 (not_2_out, d_ff_15_qn);
  not not_3 (not_3_out, ACLK);
  D_Flip_Flop d_ff_3 (.clk(nACLK), .D(d_ff_5_q), .Qn(d_ff_3_qn));  // open: Q, preset, en, reset
  not not_4 (not_4_out, PHI1);
  nor nor_2 (DSTEP, d_ff_1_q, nFLOAD, d_ff_2_q);
  S_R_Flip_Flop #(.trigger("high")) s_r_ff_1 (
    .S(or_1_out), .clk(1'b1), .R(BLOAD), .Q(s_r_ff_1_q));  // open: Qn, preset, reset, en
  and and_1 (and_1_out, ACLK, W4015);
  or or_2 (or_2_out, Res, nor_5_out);
  D_Flip_Flop d_ff_4 (.clk(not_3_out), .D(d_ff_3_qn), .Qn(d_ff_4_qn));  // open: Q, preset, en, reset
  nand nand_1 (nand_1_out, not_4_out, R_W);
  not not_5 (not_5_out, NOUT);
  D_Flip_Flop #(.trigger("high")) d_ff_5 (
    .clk(and_1_out), .D(D4), .Q(d_ff_5_q), .Qn(d_ff_5_qn), .reset(or_2_out));  // open: preset, en
  D_Flip_Flop d_ff_6 (.clk(nACLK), .D(d_ff_4_qn), .Q(d_ff_6_q));  // open: Qn, preset, en, reset
  D_Flip_Flop d_ff_7 (.clk(nACLK), .D(d_ff_4_qn), .Qn(d_ff_7_qn));  // open: Q, preset, en, reset
  Counter counter_1 (.clk(DSTEP));  // open: load, D, count, Q, carry, clr
  or or_3 (or_3_out, Res, nor_3_out);
  S_R_Flip_Flop #(.trigger("high")) s_r_ff_2 (
    .S(PCM), .clk(1'b1), .R(or_3_out), .Qn(s_r_ff_2_qn));  // open: Q, preset, reset, en
  D_Flip_Flop d_ff_8 (.clk(nACLK), .D(s_r_ff_2_qn), .Q(d_ff_8_q));  // open: Qn, preset, en, reset
  not not_6 (not_6_out, not_3_out);
  nor nor_3 (nor_3_out, d_ff_8_q, not_6_out);
  nor nor_4 (PCM, PHI1, Z4);
  not not_7 (not_7_out, nor_3_out);
  D_Flip_Flop d_ff_9 (.clk(nACLK), .D(SOUT), .Q(d_ff_9_q));  // open: Qn, preset, en, reset
  D_Flip_Flop d_ff_10 (.clk(nACLK), .D(SOUT), .Qn(d_ff_10_qn));  // open: Q, preset, en, reset
  D_Flip_Flop d_ff_11 (.clk(nACLK), .D(SOUT), .Q(d_ff_11_q));  // open: Qn, preset, en, reset
  not not_8 (not_8_out, s_r_ff_6_qn);
  and and_2 (and_2_out, d_ff_13_q, nACLK);
  nor nor_5 (nor_5_out, d_ff_10_qn, LOOP, not_7_out);
  nor nor_6 (SSTEP, not_7_out, nor_7_out, d_ff_9_q);
  nor nor_7 (nor_7_out, ACLK, d_ff_3_qn, d_ff_6_q);
  or or_4 (or_4_out, Res, d_ff_7_qn, not_8_out);
  S_R_Flip_Flop #(.trigger("high")) s_r_ff_3 (
    .S(not_3_out), .clk(1'b1), .R(and_2_out), .Qn(s_r_ff_3_qn));  // open: Q, preset, reset, en
  S_R_Flip_Flop #(.trigger("high")) s_r_ff_4 (
    .S(or_4_out), .clk(1'b1), .R(nor_8_out), .Qn(s_r_ff_4_qn));  // open: Q, preset, reset, en
  S_R_Flip_Flop #(.trigger("high")) s_r_ff_5 (
    .S(or_5_out), .clk(1'b1), .R(nor_5_out), .Q(s_r_ff_5_q));  // open: Qn, preset, reset, en
  or or_5 (or_5_out, W4015, Res, ENIRQ);
  nor nor_8 (nor_8_out, d_ff_7_qn, not_8_out, nand_1_out);
  not not_9 (Z4, s_r_ff_3_qn);
  nor nor_9 (out_21, s_r_ff_4_qn, s_r_ff_3_qn);
  or or_6 (or_6_out, Res, BLOAD);
  S_R_Flip_Flop #(.trigger("high")) s_r_ff_6 (
    .S(PCM), .clk(1'b1), .R(or_6_out), .Q(s_r_ff_6_q), .Qn(s_r_ff_6_qn));  // open: preset, reset, en
  not not_10 (not_10_out, nR4015);
  and and_3 (and_3_out, nor_3_out, d_ff_11_q);
  D_Flip_Flop d_ff_12 (.clk(not_3_out), .D(s_r_ff_4_qn), .Qn(d_ff_12_qn));  // open: Q, preset, en, reset
  D_Flip_Flop d_ff_13 (.clk(not_3_out), .D(s_r_ff_4_qn), .Q(d_ff_13_q));  // open: Qn, preset, en, reset
  assign D4_2 = not_10_out ? ~d_ff_5_qn : 1'bz;  // Controlled_Inverter controlled_inverter_1
  nor nor_10 (nDMCINT, ENIRQ, s_r_ff_5_q);
  assign D7 = not_10_out ? ~s_r_ff_5_q : 1'bz;  // Controlled_Inverter controlled_inverter_2
  not not_11 (SLOAD, nor_11_out);
  nor nor_11 (nor_11_out, nor_7_out, and_3_out);
  D_Flip_Flop d_ff_14 (.clk(nACLK), .D(d_ff_12_qn), .Qn(RUNDMC));  // open: Q, preset, en, reset
  D_Flip_Flop d_ff_15 (.clk(nACLK), .D(s_r_ff_6_q), .Qn(d_ff_15_qn));  // open: Q, preset, en, reset
  not not_12 (NSTEP, nFLOAD);
  nor nor_12 (BLOAD, nFLOAD, d_ff_15_qn, NOUT);
  nor nor_13 (BSTEP, nFLOAD, not_5_out);
  Counter counter_2 (.Q(counter_2_q), .clk(SSTEP), .clr(BLOAD));  // open: load, D, count, carry
  Register_part register_1 (.D(counter_2_q), .clk(BLOAD));  // open: en, Q, clr

  // Notes on the sheet:
  //   Inv1
  //   Nor5
  //   DL3
  //   DL12
  //   RS2
  //   Inv5
  //   DL6
  //   Inv4
  //   Nor8
  //   DL11
  //   Inv6
  //   DL5
  //   DL4
  //   RS3
  //   DL10
  //   Inv7
  //   DL14
  //   Nor8
  //   Nor10
  //   Inv10
  //   z1
  //   z2
  //   z3
  //   DL1
  //   DL2
  //   Inv3
  //   Nor2
  //   Nor11
  //   Nor3
  //   RS5
  //   RS6
  //   Nor4
  //   Nor6
  //   RS1
  //   DL9
  //   DL8
  //   RS4
  //   Nor+and
  //   DL7
  //   DL13
  //   Nor1
  //   Inv2
  //   Nor7
  //   Nor9
endmodule

module Sample_bit_counter (
  input  nACLK,
  input  NSTEP,
  input  RES,
  output NOUT
);

  wire d_ff_1_q, d_ff_1_qn, d_ff_2_q, d_ff_2_qn, d_ff_3_q, d_ff_3_qn, d_ff_4_qn, d_ff_5_qn, d_ff_6_qn,
       multiplexer_1_out, multiplexer_2_out, multiplexer_3_out, nor_1_out, nor_2_out, nor_3_out, not_1_out,
       not_2_out, not_3_out;

  D_Flip_Flop d_ff_1 (.clk(NSTEP), .D(d_ff_4_qn), .Q(d_ff_1_q), .Qn(d_ff_1_qn), .reset(RES));  // open: preset, en
  not not_1 (not_1_out, 1'b1);
  D_Flip_Flop d_ff_2 (.clk(NSTEP), .D(d_ff_5_qn), .Q(d_ff_2_q), .Qn(d_ff_2_qn), .reset(RES));  // open: preset, en
  not not_2 (not_2_out, nor_1_out);
  D_Flip_Flop d_ff_3 (.clk(NSTEP), .D(d_ff_6_qn), .Q(d_ff_3_q), .Qn(d_ff_3_qn), .reset(RES));  // open: preset, en
  not not_3 (not_3_out, nor_2_out);
  D_Flip_Flop d_ff_4 (.clk(nACLK), .D(multiplexer_1_out), .Qn(d_ff_4_qn));  // open: Q, preset, en, reset
  Multiplexer multiplexer_1 (.in0(d_ff_1_qn), .in1(d_ff_1_q), .out(multiplexer_1_out), .sel(1'b1));  // open: en
  D_Flip_Flop d_ff_5 (.clk(nACLK), .D(multiplexer_2_out), .Qn(d_ff_5_qn));  // open: Q, preset, en, reset
  Multiplexer multiplexer_2 (.in0(d_ff_2_qn), .in1(d_ff_2_q), .out(multiplexer_2_out), .sel(nor_1_out));  // open: en
  D_Flip_Flop d_ff_6 (.clk(nACLK), .D(multiplexer_3_out), .Qn(d_ff_6_qn));  // open: Q, preset, en, reset
  Multiplexer multiplexer_3 (.in0(d_ff_3_qn), .in1(d_ff_3_q), .out(multiplexer_3_out), .sel(nor_2_out));  // open: en
  nor nor_1 (nor_1_out, d_ff_1_qn, not_1_out);
  nor nor_2 (nor_2_out, d_ff_2_qn, not_2_out);
  nor nor_3 (nor_3_out, d_ff_3_qn, not_3_out);
  D_Flip_Flop d_ff_7 (.clk(nACLK), .D(nor_3_out), .Qn(NOUT));  // open: Q, preset, en, reset
endmodule

module Address_counter (
  input  nACLK,
  input  SLOAD,
  input  SSTEP,
  input  RES,
  input  LDMC6,
  input  LDMC7,
  input  LDMC8,
  input  LDMC9,
  input  LDMC10,
  input  LDMC11,
  input  LDMC12,
  input  LDMC13,
  output DMC_A0,
  output DMC_A1,
  output DMC_A2,
  output DMC_A3,
  output DMC_A4,
  output DMC_A5,
  output DMC_A6,
  output DMC_A7,
  output DMC_A8,
  output DMC_A9,
  output DMC_A10,
  output DMC_A11,
  output DMC_A12,
  output DMC_A13,
  output DMC_A14
);

  wire and_1_out, and_2_out, and_3_out, and_4_out, and_5_out, and_6_out, and_7_out, and_8_out, and_9_out,
       and_10_out, and_11_out, and_12_out, and_13_out, and_14_out, and_15_out, and_16_out, and_17_out,
       d_ff_1_qn, d_ff_2_qn, d_ff_3_qn, d_ff_4_qn, d_ff_5_qn, d_ff_6_qn, d_ff_7_qn, d_ff_8_qn, d_ff_9_qn,
       d_ff_10_qn, d_ff_11_qn, d_ff_12_qn, d_ff_13_qn, d_ff_14_qn, d_ff_15_qn, d_ff_16_qn, d_ff_17_qn,
       d_ff_18_qn, d_ff_19_qn, d_ff_20_qn, d_ff_21_qn, d_ff_22_qn, d_ff_23_qn, d_ff_24_qn, d_ff_25_qn,
       d_ff_26_qn, d_ff_27_qn, d_ff_28_qn, d_ff_29_qn, d_ff_30_qn, multiplexer_1_out, multiplexer_2_out,
       multiplexer_3_out, multiplexer_4_out, multiplexer_5_out, multiplexer_6_out, multiplexer_7_out,
       multiplexer_8_out, multiplexer_9_out, multiplexer_10_out, multiplexer_11_out, multiplexer_12_out,
       multiplexer_13_out, multiplexer_14_out, multiplexer_15_out, nor_1_out, nor_2_out, nor_3_out,
       nor_4_out, nor_5_out, nor_6_out, nor_7_out, nor_8_out, nor_9_out, nor_10_out, nor_11_out, nor_12_out,
       nor_13_out, nor_14_out, not_1_out, not_2_out, not_3_out, not_4_out, not_5_out, not_6_out, not_7_out,
       not_8_out, not_9_out, not_10_out, not_11_out, not_12_out, not_13_out, not_14_out, not_15_out,
       not_16_out, not_17_out, not_18_out, not_19_out, not_20_out, not_21_out, not_22_out, or_1_out,
       or_2_out, or_3_out, or_4_out, or_5_out, or_6_out, or_7_out, or_8_out, or_9_out, or_10_out, or_11_out,
       or_12_out, or_13_out, or_14_out;

  not not_1 (not_1_out, LDMC6);
  not not_2 (not_2_out, LDMC7);
  not not_3 (not_3_out, LDMC8);
  not not_4 (not_4_out, LDMC9);
  not not_5 (not_5_out, LDMC10);
  not not_6 (not_6_out, LDMC11);
  not not_7 (not_7_out, LDMC12);
  not not_8 (not_8_out, LDMC13);
  D_Flip_Flop d_ff_1 (.clk(SSTEP), .D(d_ff_16_qn), .Q(DMC_A0), .Qn(d_ff_1_qn), .reset(or_1_out));  // open: preset, en
  or or_1 (or_1_out, SLOAD, RES);
  D_Flip_Flop d_ff_2 (.clk(SSTEP), .D(d_ff_17_qn), .Q(DMC_A1), .Qn(d_ff_2_qn), .reset(or_2_out));  // open: preset, en
  or or_2 (or_2_out, SLOAD, RES);
  D_Flip_Flop d_ff_3 (.clk(SSTEP), .D(d_ff_18_qn), .Q(DMC_A2), .Qn(d_ff_3_qn), .reset(or_3_out));  // open: preset, en
  or or_3 (or_3_out, SLOAD, RES);
  D_Flip_Flop d_ff_4 (.clk(SSTEP), .D(d_ff_19_qn), .Q(DMC_A3), .Qn(d_ff_4_qn), .reset(or_4_out));  // open: preset, en
  or or_4 (or_4_out, SLOAD, RES);
  D_Flip_Flop d_ff_5 (.clk(SSTEP), .D(d_ff_20_qn), .Q(DMC_A4), .Qn(d_ff_5_qn), .reset(or_5_out));  // open: preset, en
  or or_5 (or_5_out, SLOAD, RES);
  D_Flip_Flop d_ff_6 (.clk(SSTEP), .D(d_ff_21_qn), .Q(DMC_A5), .Qn(d_ff_6_qn), .reset(or_6_out));  // open: preset, en
  or or_6 (or_6_out, SLOAD, RES);
  D_Flip_Flop d_ff_7 (
    .clk(SSTEP), .D(d_ff_22_qn), .Q(DMC_A6), .Qn(d_ff_7_qn), .preset(and_1_out), .reset(or_7_out));  // open: en
  or or_7 (or_7_out, and_2_out, RES);
  and and_1 (and_1_out, LDMC6, SLOAD);
  and and_2 (and_2_out, SLOAD, not_1_out);
  D_Flip_Flop d_ff_8 (
    .clk(SSTEP), .D(d_ff_23_qn), .Q(DMC_A7), .Qn(d_ff_8_qn), .preset(and_3_out), .reset(or_8_out));  // open: en
  or or_8 (or_8_out, and_4_out, RES);
  and and_3 (and_3_out, LDMC7, SLOAD);
  and and_4 (and_4_out, SLOAD, not_2_out);
  D_Flip_Flop d_ff_9 (
    .clk(SSTEP), .D(d_ff_24_qn), .Q(DMC_A8), .Qn(d_ff_9_qn), .preset(and_5_out), .reset(or_9_out));  // open: en
  and and_5 (and_5_out, LDMC8, SLOAD);
  or or_9 (or_9_out, and_6_out, RES);
  and and_6 (and_6_out, SLOAD, not_3_out);
  D_Flip_Flop d_ff_10 (
    .clk(SSTEP), .D(d_ff_25_qn), .Q(DMC_A9), .Qn(d_ff_10_qn), .preset(and_7_out), .reset(or_10_out));  // open: en
  or or_10 (or_10_out, and_8_out, RES);
  and and_7 (and_7_out, LDMC9, SLOAD);
  and and_8 (and_8_out, SLOAD, not_4_out);
  D_Flip_Flop d_ff_11 (
    .clk(SSTEP), .D(d_ff_26_qn), .Q(DMC_A10), .Qn(d_ff_11_qn), .preset(and_9_out), .reset(or_11_out));  // open: en
  or or_11 (or_11_out, and_10_out, RES);
  and and_9 (and_9_out, LDMC10, SLOAD);
  and and_10 (and_10_out, SLOAD, not_5_out);
  D_Flip_Flop d_ff_12 (
    .clk(SSTEP), .D(d_ff_27_qn), .Q(DMC_A11), .Qn(d_ff_12_qn), .preset(and_11_out), .reset(or_12_out));  // open: en
  and and_11 (and_11_out, LDMC11, SLOAD);
  or or_12 (or_12_out, and_12_out, RES);
  and and_12 (and_12_out, SLOAD, not_6_out);
  D_Flip_Flop d_ff_13 (
    .clk(SSTEP), .D(d_ff_28_qn), .Q(DMC_A12), .Qn(d_ff_13_qn), .preset(and_13_out), .reset(or_13_out));  // open: en
  and and_13 (and_13_out, LDMC12, SLOAD);
  or or_13 (or_13_out, and_14_out, RES);
  and and_14 (and_14_out, SLOAD, not_7_out);
  D_Flip_Flop d_ff_14 (
    .clk(SSTEP), .D(d_ff_29_qn), .Q(DMC_A13), .Qn(d_ff_14_qn), .preset(and_15_out), .reset(or_14_out));  // open: en
  or or_14 (or_14_out, and_16_out, RES);
  and and_15 (and_15_out, LDMC13, SLOAD);
  and and_16 (and_16_out, SLOAD, not_8_out);
  D_Flip_Flop d_ff_15 (
    .clk(SSTEP), .D(d_ff_30_qn), .Q(DMC_A14), .Qn(d_ff_15_qn), .preset(and_17_out), .reset(RES));  // open: en
  and and_17 (and_17_out, SLOAD, 1'b1);
  Multiplexer multiplexer_1 (.in0(d_ff_1_qn), .in1(DMC_A0), .out(multiplexer_1_out), .sel(1'b1));  // open: en
  not not_9 (not_9_out, 1'b1);
  Multiplexer multiplexer_2 (.in0(d_ff_2_qn), .in1(DMC_A1), .out(multiplexer_2_out), .sel(nor_1_out));  // open: en
  not not_10 (not_10_out, nor_1_out);
  Multiplexer multiplexer_3 (.in0(d_ff_3_qn), .in1(DMC_A2), .out(multiplexer_3_out), .sel(nor_2_out));  // open: en
  not not_11 (not_11_out, nor_2_out);
  Multiplexer multiplexer_4 (.in0(d_ff_4_qn), .in1(DMC_A3), .out(multiplexer_4_out), .sel(nor_3_out));  // open: en
  not not_12 (not_12_out, nor_3_out);
  Multiplexer multiplexer_5 (.in0(d_ff_5_qn), .in1(DMC_A4), .out(multiplexer_5_out), .sel(nor_4_out));  // open: en
  not not_13 (not_13_out, nor_4_out);
  Multiplexer multiplexer_6 (.in0(d_ff_6_qn), .in1(DMC_A5), .out(multiplexer_6_out), .sel(nor_5_out));  // open: en
  not not_14 (not_14_out, nor_5_out);
  Multiplexer multiplexer_7 (.in0(d_ff_7_qn), .in1(DMC_A6), .out(multiplexer_7_out), .sel(nor_6_out));  // open: en
  not not_15 (not_15_out, nor_6_out);
  Multiplexer multiplexer_8 (.in0(d_ff_8_qn), .in1(DMC_A7), .out(multiplexer_8_out), .sel(nor_7_out));  // open: en
  not not_16 (not_16_out, nor_7_out);
  Multiplexer multiplexer_9 (.in0(d_ff_9_qn), .in1(DMC_A8), .out(multiplexer_9_out), .sel(nor_8_out));  // open: en
  not not_17 (not_17_out, nor_8_out);
  Multiplexer multiplexer_10 (.in0(d_ff_10_qn), .in1(DMC_A9), .out(multiplexer_10_out), .sel(nor_9_out));  // open: en
  not not_18 (not_18_out, nor_9_out);
  Multiplexer multiplexer_11 (.in0(d_ff_11_qn), .in1(DMC_A10), .out(multiplexer_11_out), .sel(nor_10_out));  // open: en
  not not_19 (not_19_out, nor_10_out);
  Multiplexer multiplexer_12 (.in0(d_ff_12_qn), .in1(DMC_A11), .out(multiplexer_12_out), .sel(nor_11_out));  // open: en
  not not_20 (not_20_out, nor_11_out);
  Multiplexer multiplexer_13 (.in0(d_ff_13_qn), .in1(DMC_A12), .out(multiplexer_13_out), .sel(nor_12_out));  // open: en
  not not_21 (not_21_out, nor_12_out);
  Multiplexer multiplexer_14 (.in0(d_ff_14_qn), .in1(DMC_A13), .out(multiplexer_14_out), .sel(nor_13_out));  // open: en
  not not_22 (not_22_out, nor_13_out);
  Multiplexer multiplexer_15 (.in0(d_ff_15_qn), .in1(DMC_A14), .out(multiplexer_15_out), .sel(nor_14_out));  // open: en
  D_Flip_Flop d_ff_16 (.clk(nACLK), .D(multiplexer_1_out), .Qn(d_ff_16_qn));  // open: Q, preset, en, reset
  D_Flip_Flop d_ff_17 (.clk(nACLK), .D(multiplexer_2_out), .Qn(d_ff_17_qn));  // open: Q, preset, en, reset
  D_Flip_Flop d_ff_18 (.clk(nACLK), .D(multiplexer_3_out), .Qn(d_ff_18_qn));  // open: Q, preset, en, reset
  D_Flip_Flop d_ff_19 (.clk(nACLK), .D(multiplexer_4_out), .Qn(d_ff_19_qn));  // open: Q, preset, en, reset
  D_Flip_Flop d_ff_20 (.clk(nACLK), .D(multiplexer_5_out), .Qn(d_ff_20_qn));  // open: Q, preset, en, reset
  D_Flip_Flop d_ff_21 (.clk(nACLK), .D(multiplexer_6_out), .Qn(d_ff_21_qn));  // open: Q, preset, en, reset
  D_Flip_Flop d_ff_22 (.clk(nACLK), .D(multiplexer_7_out), .Qn(d_ff_22_qn));  // open: Q, preset, en, reset
  D_Flip_Flop d_ff_23 (.clk(nACLK), .D(multiplexer_8_out), .Qn(d_ff_23_qn));  // open: Q, preset, en, reset
  D_Flip_Flop d_ff_24 (.clk(nACLK), .D(multiplexer_9_out), .Qn(d_ff_24_qn));  // open: Q, preset, en, reset
  D_Flip_Flop d_ff_25 (.clk(nACLK), .D(multiplexer_10_out), .Qn(d_ff_25_qn));  // open: Q, preset, en, reset
  D_Flip_Flop d_ff_26 (.clk(nACLK), .D(multiplexer_11_out), .Qn(d_ff_26_qn));  // open: Q, preset, en, reset
  D_Flip_Flop d_ff_27 (.clk(nACLK), .D(multiplexer_12_out), .Qn(d_ff_27_qn));  // open: Q, preset, en, reset
  D_Flip_Flop d_ff_28 (.clk(nACLK), .D(multiplexer_13_out), .Qn(d_ff_28_qn));  // open: Q, preset, en, reset
  D_Flip_Flop d_ff_29 (.clk(nACLK), .D(multiplexer_14_out), .Qn(d_ff_29_qn));  // open: Q, preset, en, reset
  D_Flip_Flop d_ff_30 (.clk(nACLK), .D(multiplexer_15_out), .Qn(d_ff_30_qn));  // open: Q, preset, en, reset
  nor nor_1 (nor_1_out, d_ff_1_qn, not_9_out);
  nor nor_2 (nor_2_out, d_ff_2_qn, not_10_out);
  nor nor_3 (nor_3_out, d_ff_3_qn, not_11_out);
  nor nor_4 (nor_4_out, d_ff_4_qn, not_12_out);
  nor nor_5 (nor_5_out, d_ff_5_qn, not_13_out);
  nor nor_6 (nor_6_out, d_ff_6_qn, not_14_out);
  nor nor_7 (nor_7_out, d_ff_7_qn, not_15_out);
  nor nor_8 (nor_8_out, d_ff_8_qn, not_16_out);
  nor nor_9 (nor_9_out, d_ff_9_qn, not_17_out);
  nor nor_10 (nor_10_out, d_ff_10_qn, not_18_out);
  nor nor_11 (nor_11_out, d_ff_11_qn, not_19_out);
  nor nor_12 (nor_12_out, d_ff_12_qn, not_20_out);
  nor nor_13 (nor_13_out, d_ff_13_qn, not_21_out);
  nor nor_14 (nor_14_out, d_ff_14_qn, not_22_out);
  // Probe on {1'b1, DMC_A14, DMC_A13, DMC_A12, DMC_A11, DMC_A10, DMC_A9, DMC_A8, DMC_A7, DMC_A6, DMC_A5, DMC_A4, DMC_A3, DMC_A2, DMC_A1, DMC_A0}
endmodule

module sample_lenght_counter (
  input  nACLK,
  input  SLOAD,
  input  SSTEP,
  input  RES,
  input  LSC0,
  input  LSC1,
  input  LSC2,
  input  LSC3,
  input  LSC4,
  input  LSC5,
  input  LSC6,
  input  LSC7,
  output SOUT
);

  wire and_1_out, and_2_out, and_3_out, and_4_out, and_5_out, and_6_out, and_7_out, and_8_out, and_9_out,
       and_10_out, and_11_out, and_12_out, and_13_out, and_14_out, and_15_out, and_16_out, d_ff_1_qn,
       d_ff_2_qn, d_ff_3_qn, d_ff_4_qn, d_ff_5_qn, d_ff_6_qn, d_ff_7_qn, d_ff_8_qn, d_ff_9_qn, d_ff_10_qn,
       d_ff_11_qn, d_ff_12_qn, d_ff_13_qn, d_ff_14_qn, d_ff_15_qn, d_ff_16_qn, d_ff_17_qn, d_ff_18_qn,
       d_ff_19_qn, d_ff_20_qn, d_ff_21_qn, d_ff_22_qn, d_ff_23_qn, d_ff_24_qn, d_ff_25_q, d_ff_25_qn,
       multiplexer_1_out, multiplexer_2_out, multiplexer_3_out, multiplexer_4_out, multiplexer_5_out,
       multiplexer_6_out, multiplexer_7_out, multiplexer_8_out, multiplexer_9_out, multiplexer_10_out,
       multiplexer_11_out, multiplexer_12_out, nor_1_out, nor_2_out, nor_3_out, nor_4_out, nor_5_out,
       nor_6_out, nor_7_out, nor_8_out, nor_9_out, nor_10_out, nor_11_out, not_1_out, not_2_out, not_3_out,
       not_4_out, not_5_out, not_6_out, not_7_out, not_8_out, not_9_out, not_10_out, not_11_out, not_12_out,
       not_13_out, not_14_out, not_15_out, not_16_out, not_17_out, not_18_out, not_19_out, not_20_out,
       not_21_out, or_1_out, or_2_out, or_3_out, or_4_out, or_5_out, or_6_out, or_7_out, or_8_out, or_9_out,
       or_10_out, or_11_out, or_12_out, undriven, undriven_2, undriven_3;
  wire [11:0] counter_1_q, d_ff_1_q;

  not not_1 (not_1_out, LSC0);
  not not_2 (not_2_out, LSC1);
  not not_3 (not_3_out, LSC2);
  not not_4 (not_4_out, LSC3);
  not not_5 (not_5_out, LSC4);
  not not_6 (not_6_out, LSC5);
  not not_7 (not_7_out, LSC6);
  not not_8 (not_8_out, LSC7);
  D_Flip_Flop d_ff_1 (
    .clk(SSTEP), .D(d_ff_13_qn), .Q(d_ff_1_q[0]), .Qn(d_ff_1_qn), .reset(or_1_out));  // open: preset, en
  or or_1 (or_1_out, SLOAD, RES);
  D_Flip_Flop d_ff_2 (
    .clk(SSTEP), .D(d_ff_14_qn), .Q(d_ff_1_q[1]), .Qn(d_ff_2_qn), .reset(or_2_out));  // open: preset, en
  or or_2 (or_2_out, SLOAD, RES);
  D_Flip_Flop d_ff_3 (
    .clk(SSTEP), .D(d_ff_15_qn), .Q(d_ff_1_q[2]), .Qn(d_ff_3_qn), .reset(or_3_out));  // open: preset, en
  or or_3 (or_3_out, SLOAD, RES);
  D_Flip_Flop d_ff_4 (
    .clk(SSTEP), .D(d_ff_16_qn), .Q(d_ff_1_q[3]), .Qn(d_ff_4_qn), .reset(or_4_out));  // open: preset, en
  or or_4 (or_4_out, SLOAD, RES);
  D_Flip_Flop d_ff_5 (
    .clk(SSTEP), .D(d_ff_17_qn), .Q(d_ff_1_q[4]), .Qn(d_ff_5_qn), .preset(and_1_out), .reset(or_5_out));  // open: en
  and and_1 (and_1_out, LSC0, SLOAD);
  or or_5 (or_5_out, and_2_out, RES);
  and and_2 (and_2_out, SLOAD, not_1_out);
  D_Flip_Flop d_ff_6 (
    .clk(SSTEP), .D(d_ff_18_qn), .Q(d_ff_1_q[5]), .Qn(d_ff_6_qn), .preset(and_3_out), .reset(or_6_out));  // open: en
  and and_3 (and_3_out, LSC1, SLOAD);
  or or_6 (or_6_out, and_4_out, RES);
  and and_4 (and_4_out, SLOAD, not_2_out);
  D_Flip_Flop d_ff_7 (
    .clk(SSTEP), .D(d_ff_19_qn), .Q(d_ff_1_q[6]), .Qn(d_ff_7_qn), .preset(and_5_out), .reset(or_7_out));  // open: en
  and and_5 (and_5_out, LSC2, SLOAD);
  or or_7 (or_7_out, and_6_out, RES);
  and and_6 (and_6_out, SLOAD, not_3_out);
  D_Flip_Flop d_ff_8 (
    .clk(SSTEP), .D(d_ff_20_qn), .Q(d_ff_1_q[7]), .Qn(d_ff_8_qn), .preset(and_7_out), .reset(or_8_out));  // open: en
  or or_8 (or_8_out, and_8_out, RES);
  and and_7 (and_7_out, LSC3, SLOAD);
  and and_8 (and_8_out, SLOAD, not_4_out);
  D_Flip_Flop d_ff_9 (
    .clk(SSTEP), .D(d_ff_21_qn), .Q(d_ff_1_q[8]), .Qn(d_ff_9_qn), .preset(and_9_out), .reset(or_9_out));  // open: en
  or or_9 (or_9_out, and_10_out, RES);
  and and_9 (and_9_out, LSC4, SLOAD);
  and and_10 (and_10_out, SLOAD, not_5_out);
  D_Flip_Flop d_ff_10 (
    .clk(SSTEP), .D(d_ff_22_qn), .Q(d_ff_1_q[9]), .Qn(d_ff_10_qn), .preset(and_11_out), .reset(or_10_out));  // open: en
  and and_11 (and_11_out, LSC5, SLOAD);
  or or_10 (or_10_out, and_12_out, RES);
  and and_12 (and_12_out, SLOAD, not_6_out);
  D_Flip_Flop d_ff_11 (
    .clk(SSTEP), .D(d_ff_23_qn), .Q(d_ff_1_q[10]), .Qn(d_ff_11_qn), .preset(and_13_out), .reset(or_11_out));  // open: en
  or or_11 (or_11_out, and_14_out, RES);
  and and_13 (and_13_out, LSC6, SLOAD);
  and and_14 (and_14_out, SLOAD, not_7_out);
  D_Flip_Flop d_ff_12 (
    .clk(SSTEP), .D(d_ff_24_qn), .Q(d_ff_1_q[11]), .Qn(d_ff_12_qn), .preset(and_15_out), .reset(or_12_out));  // open: en
  and and_15 (and_15_out, LSC7, SLOAD);
  or or_12 (or_12_out, and_16_out, RES);
  and and_16 (and_16_out, SLOAD, not_8_out);
  Multiplexer multiplexer_1 (.in0(d_ff_1_qn), .in1(d_ff_1_q[0]), .out(multiplexer_1_out), .sel(1'b1));  // open: en
  not not_9 (not_9_out, 1'b1);
  Multiplexer multiplexer_2 (.in0(d_ff_2_qn), .in1(d_ff_1_q[1]), .out(multiplexer_2_out), .sel(nor_1_out));  // open: en
  not not_10 (not_10_out, nor_1_out);
  Multiplexer multiplexer_3 (.in0(d_ff_3_qn), .in1(d_ff_1_q[2]), .out(multiplexer_3_out), .sel(nor_2_out));  // open: en
  not not_11 (not_11_out, nor_2_out);
  Multiplexer multiplexer_4 (.in0(d_ff_4_qn), .in1(d_ff_1_q[3]), .out(multiplexer_4_out), .sel(nor_3_out));  // open: en
  not not_12 (not_12_out, nor_3_out);
  Multiplexer multiplexer_5 (.in0(d_ff_5_qn), .in1(d_ff_1_q[4]), .out(multiplexer_5_out), .sel(nor_4_out));  // open: en
  not not_13 (not_13_out, nor_4_out);
  Multiplexer multiplexer_6 (.in0(d_ff_6_qn), .in1(d_ff_1_q[5]), .out(multiplexer_6_out), .sel(nor_5_out));  // open: en
  not not_14 (not_14_out, nor_5_out);
  Multiplexer multiplexer_7 (.in0(d_ff_7_qn), .in1(d_ff_1_q[6]), .out(multiplexer_7_out), .sel(nor_6_out));  // open: en
  not not_15 (not_15_out, nor_6_out);
  Multiplexer multiplexer_8 (.in0(d_ff_8_qn), .in1(d_ff_1_q[7]), .out(multiplexer_8_out), .sel(nor_7_out));  // open: en
  not not_16 (not_16_out, nor_7_out);
  Multiplexer multiplexer_9 (.in0(d_ff_9_qn), .in1(d_ff_1_q[8]), .out(multiplexer_9_out), .sel(nor_8_out));  // open: en
  not not_17 (not_17_out, nor_8_out);
  Multiplexer multiplexer_10 (
    .in0(d_ff_10_qn), .in1(d_ff_1_q[9]), .out(multiplexer_10_out), .sel(nor_9_out));  // open: en
  not not_18 (not_18_out, nor_9_out);
  Multiplexer multiplexer_11 (
    .in0(d_ff_11_qn), .in1(d_ff_1_q[10]), .out(multiplexer_11_out), .sel(nor_10_out));  // open: en
  not not_19 (not_19_out, nor_10_out);
  Multiplexer multiplexer_12 (
    .in0(d_ff_12_qn), .in1(d_ff_1_q[11]), .out(multiplexer_12_out), .sel(nor_11_out));  // open: en
  not not_20 (not_20_out, nor_11_out);
  D_Flip_Flop d_ff_13 (.clk(nACLK), .D(multiplexer_1_out), .Qn(d_ff_13_qn));  // open: Q, preset, en, reset
  D_Flip_Flop d_ff_14 (.clk(nACLK), .D(multiplexer_2_out), .Qn(d_ff_14_qn));  // open: Q, preset, en, reset
  D_Flip_Flop d_ff_15 (.clk(nACLK), .D(multiplexer_3_out), .Qn(d_ff_15_qn));  // open: Q, preset, en, reset
  D_Flip_Flop d_ff_16 (.clk(nACLK), .D(multiplexer_4_out), .Qn(d_ff_16_qn));  // open: Q, preset, en, reset
  D_Flip_Flop d_ff_17 (.clk(nACLK), .D(multiplexer_5_out), .Qn(d_ff_17_qn));  // open: Q, preset, en, reset
  D_Flip_Flop d_ff_18 (.clk(nACLK), .D(multiplexer_6_out), .Qn(d_ff_18_qn));  // open: Q, preset, en, reset
  D_Flip_Flop d_ff_19 (.clk(nACLK), .D(multiplexer_7_out), .Qn(d_ff_19_qn));  // open: Q, preset, en, reset
  D_Flip_Flop d_ff_20 (.clk(nACLK), .D(multiplexer_8_out), .Qn(d_ff_20_qn));  // open: Q, preset, en, reset
  D_Flip_Flop d_ff_21 (.clk(nACLK), .D(multiplexer_9_out), .Qn(d_ff_21_qn));  // open: Q, preset, en, reset
  D_Flip_Flop d_ff_22 (.clk(nACLK), .D(multiplexer_10_out), .Qn(d_ff_22_qn));  // open: Q, preset, en, reset
  D_Flip_Flop d_ff_23 (.clk(nACLK), .D(multiplexer_11_out), .Qn(d_ff_23_qn));  // open: Q, preset, en, reset
  D_Flip_Flop d_ff_24 (.clk(nACLK), .D(multiplexer_12_out), .Qn(d_ff_24_qn));  // open: Q, preset, en, reset
  nor nor_1 (nor_1_out, d_ff_1_q[0], not_9_out);
  nor nor_2 (nor_2_out, d_ff_1_q[1], not_10_out);
  nor nor_3 (nor_3_out, d_ff_1_q[2], not_11_out);
  nor nor_4 (nor_4_out, d_ff_1_q[3], not_12_out);
  nor nor_5 (nor_5_out, d_ff_1_q[4], not_13_out);
  nor nor_6 (nor_6_out, d_ff_1_q[5], not_14_out);
  nor nor_7 (nor_7_out, d_ff_1_q[6], not_15_out);
  nor nor_8 (nor_8_out, d_ff_1_q[7], not_16_out);
  nor nor_9 (nor_9_out, d_ff_1_q[8], not_17_out);
  nor nor_10 (nor_10_out, d_ff_1_q[9], not_18_out);
  nor nor_11 (nor_11_out, d_ff_1_q[10], not_19_out);
  nor nor_12 (SOUT, d_ff_1_q[11], not_20_out);
  not not_21 (not_21_out, undriven_2);
  Counter #(.width(12), .max('hfff)) counter_1 (
    .Q(counter_1_q), .clk(undriven), .clr(not_21_out));  // open: load, D, count, carry
  D_Flip_Flop #(.trigger("high")) d_ff_25 (
    .clk(undriven), .D(SOUT), .Q(d_ff_25_q), .Qn(d_ff_25_qn), .reset(undriven_3));  // open: preset, en
  // Probe on d_ff_1_q
  Register_part #(.width(12), .trigger("high")) register_1 (
    .D(counter_1_q), .clk(d_ff_25_q), .clr(undriven_3));  // open: en, Q
endmodule

module Dmc_output_counter (
  input  DL0,
  input  nACLK,
  input  ACLK,
  input  DL1,
  input  W4011,
  input  DSTEP,
  input  RES,
  input  BOUT,
  input  DL2,
  input  DL3,
  input  DL4,
  input  DL5,
  input  DL6,
  output DMC0,
  output DMC1,
  output DMC2,
  output DMC3,
  output DMC4,
  output DMC5,
  output DMC6,
  output DOUT
);

  wire and_1_out, controlled_buffer_1_out, controlled_buffer_3_out, controlled_buffer_5_out,
       controlled_buffer_7_out, controlled_buffer_9_out, controlled_buffer_11_out, d_ff_2_qn, d_ff_3_qn,
       d_ff_4_qn, d_ff_5_qn, d_ff_6_qn, d_ff_7_qn, d_ff_8_qn, d_ff_9_qn, d_ff_10_qn, d_ff_11_qn, d_ff_12_qn,
       d_ff_13_qn, multiplexer_1_out, multiplexer_2_out, multiplexer_3_out, multiplexer_4_out,
       multiplexer_5_out, multiplexer_6_out, multiplexer_7_out, multiplexer_8_out, multiplexer_9_out,
       multiplexer_10_out, multiplexer_11_out, multiplexer_12_out, nor_1_out, nor_2_out, nor_3_out,
       nor_4_out, nor_5_out, not_1_out, not_2_out, not_3_out, not_4_out, not_5_out, not_6_out;

  and and_1 (and_1_out, W4011, ACLK);
  assign controlled_buffer_1_out = W4011 ? DL1 : 1'bz;  // Controlled_Buffer controlled_buffer_1
  assign controlled_buffer_1_out = DSTEP ? d_ff_8_qn : 1'bz;  // Controlled_Buffer controlled_buffer_2
  assign controlled_buffer_3_out = W4011 ? DL2 : 1'bz;  // Controlled_Buffer controlled_buffer_3
  assign controlled_buffer_3_out = DSTEP ? d_ff_9_qn : 1'bz;  // Controlled_Buffer controlled_buffer_4
  assign controlled_buffer_5_out = W4011 ? DL3 : 1'bz;  // Controlled_Buffer controlled_buffer_5
  assign controlled_buffer_5_out = DSTEP ? d_ff_10_qn : 1'bz;  // Controlled_Buffer controlled_buffer_6
  assign controlled_buffer_7_out = W4011 ? DL4 : 1'bz;  // Controlled_Buffer controlled_buffer_7
  assign controlled_buffer_7_out = DSTEP ? d_ff_11_qn : 1'bz;  // Controlled_Buffer controlled_buffer_8
  assign controlled_buffer_9_out = W4011 ? DL5 : 1'bz;  // Controlled_Buffer controlled_buffer_9
  assign controlled_buffer_9_out = DSTEP ? d_ff_12_qn : 1'bz;  // Controlled_Buffer controlled_buffer_10
  assign controlled_buffer_11_out = W4011 ? DL6 : 1'bz;  // Controlled_Buffer controlled_buffer_11
  assign controlled_buffer_11_out = DSTEP ? d_ff_13_qn : 1'bz;  // Controlled_Buffer controlled_buffer_12
  D_Flip_Flop #(.trigger("high")) d_ff_1 (.clk(and_1_out), .D(DL0), .Q(DMC0));  // open: Qn, preset, en, reset
  D_Flip_Flop #(.trigger("high")) d_ff_2 (
    .clk(nACLK), .D(controlled_buffer_1_out), .Q(DMC1), .Qn(d_ff_2_qn), .reset(RES));  // open: preset, en
  D_Flip_Flop #(.trigger("high")) d_ff_3 (
    .clk(nACLK), .D(controlled_buffer_3_out), .Q(DMC2), .Qn(d_ff_3_qn), .reset(RES));  // open: preset, en
  D_Flip_Flop #(.trigger("high")) d_ff_4 (
    .clk(nACLK), .D(controlled_buffer_5_out), .Q(DMC3), .Qn(d_ff_4_qn), .reset(RES));  // open: preset, en
  D_Flip_Flop #(.trigger("high")) d_ff_5 (
    .clk(nACLK), .D(controlled_buffer_7_out), .Q(DMC4), .Qn(d_ff_5_qn), .reset(RES));  // open: preset, en
  D_Flip_Flop #(.trigger("high")) d_ff_6 (
    .clk(nACLK), .D(controlled_buffer_9_out), .Q(DMC5), .Qn(d_ff_6_qn), .reset(RES));  // open: preset, en
  D_Flip_Flop #(.trigger("high")) d_ff_7 (
    .clk(nACLK), .D(controlled_buffer_11_out), .Q(DMC6), .Qn(d_ff_7_qn), .reset(RES));  // open: preset, en
  D_Flip_Flop #(.trigger("high")) d_ff_8 (
    .clk(ACLK), .D(multiplexer_1_out), .Qn(d_ff_8_qn));  // open: Q, preset, en, reset
  Multiplexer multiplexer_1 (.in0(d_ff_2_qn), .in1(DMC1), .out(multiplexer_1_out), .sel(1'b1));  // open: en
  not not_1 (not_1_out, 1'b1);
  D_Flip_Flop #(.trigger("high")) d_ff_9 (
    .clk(ACLK), .D(multiplexer_2_out), .Qn(d_ff_9_qn));  // open: Q, preset, en, reset
  Multiplexer multiplexer_2 (.in0(d_ff_3_qn), .in1(DMC2), .out(multiplexer_2_out), .sel(nor_1_out));  // open: en
  not not_2 (not_2_out, nor_1_out);
  D_Flip_Flop #(.trigger("high")) d_ff_10 (
    .clk(ACLK), .D(multiplexer_3_out), .Qn(d_ff_10_qn));  // open: Q, preset, en, reset
  Multiplexer multiplexer_3 (.in0(d_ff_4_qn), .in1(DMC3), .out(multiplexer_3_out), .sel(nor_2_out));  // open: en
  not not_3 (not_3_out, nor_2_out);
  D_Flip_Flop #(.trigger("high")) d_ff_11 (
    .clk(ACLK), .D(multiplexer_4_out), .Qn(d_ff_11_qn));  // open: Q, preset, en, reset
  Multiplexer multiplexer_4 (.in0(d_ff_5_qn), .in1(DMC4), .out(multiplexer_4_out), .sel(nor_3_out));  // open: en
  not not_4 (not_4_out, nor_3_out);
  D_Flip_Flop #(.trigger("high")) d_ff_12 (
    .clk(ACLK), .D(multiplexer_5_out), .Qn(d_ff_12_qn));  // open: Q, preset, en, reset
  Multiplexer multiplexer_5 (.in0(d_ff_6_qn), .in1(DMC5), .out(multiplexer_5_out), .sel(nor_4_out));  // open: en
  not not_5 (not_5_out, nor_4_out);
  D_Flip_Flop #(.trigger("high")) d_ff_13 (
    .clk(ACLK), .D(multiplexer_6_out), .Qn(d_ff_13_qn));  // open: Q, preset, en, reset
  Multiplexer multiplexer_6 (.in0(d_ff_7_qn), .in1(DMC6), .out(multiplexer_6_out), .sel(nor_5_out));  // open: en
  not not_6 (not_6_out, nor_5_out);
  Multiplexer multiplexer_7 (.in0(d_ff_2_qn), .in1(DMC1), .out(multiplexer_7_out), .sel(BOUT));  // open: en
  nor nor_1 (nor_1_out, multiplexer_7_out, not_1_out);
  Multiplexer multiplexer_8 (.in0(d_ff_3_qn), .in1(DMC2), .out(multiplexer_8_out), .sel(BOUT));  // open: en
  nor nor_2 (nor_2_out, multiplexer_8_out, not_2_out);
  Multiplexer multiplexer_9 (.in0(d_ff_4_qn), .in1(DMC3), .out(multiplexer_9_out), .sel(BOUT));  // open: en
  nor nor_3 (nor_3_out, multiplexer_9_out, not_3_out);
  Multiplexer multiplexer_10 (.in0(d_ff_5_qn), .in1(DMC4), .out(multiplexer_10_out), .sel(BOUT));  // open: en
  nor nor_4 (nor_4_out, multiplexer_10_out, not_4_out);
  Multiplexer multiplexer_11 (.in0(d_ff_6_qn), .in1(DMC5), .out(multiplexer_11_out), .sel(BOUT));  // open: en
  nor nor_5 (nor_5_out, multiplexer_11_out, not_5_out);
  Multiplexer multiplexer_12 (.in0(d_ff_7_qn), .in1(DMC6), .out(multiplexer_12_out), .sel(BOUT));  // open: en
  nor nor_6 (DOUT, multiplexer_12_out, not_6_out);
  // Probe on {DMC6, DMC5, DMC4, DMC3, DMC2, DMC1}
endmodule

module Sample_shift_register (
  input  ACLK,
  input  nACLK,
  input  SL0,
  input  SL1,
  input  SL2,
  input  SL3,
  input  SL4,
  input  SL5,
  input  SL6,
  input  SL7,
  input  BSTEP,
  input  BLOAD,
  input  res,
  input  PCM,
  output BOUT
);

  wire and_1_out, controlled_buffer_1_out, controlled_buffer_3_out, controlled_buffer_5_out,
       controlled_buffer_7_out, controlled_buffer_9_out, controlled_buffer_11_out, controlled_buffer_13_out,
       controlled_buffer_15_out, d_ff_1_q, d_ff_2_q, d_ff_3_q, d_ff_4_q, d_ff_5_q, d_ff_6_q, d_ff_7_q,
       d_ff_8_q, d_ff_9_qn, d_ff_10_qn, d_ff_11_qn, d_ff_12_qn, d_ff_13_qn, d_ff_14_qn, d_ff_15_qn,
       d_ff_16_qn, d_ff_18_qn, d_ff_19_qn, d_ff_20_qn, d_ff_21_qn, d_ff_22_qn, d_ff_23_qn, d_ff_24_qn;

  D_Flip_Flop #(.trigger("high")) d_ff_1 (.clk(and_1_out), .D(SL0), .Q(d_ff_1_q));  // open: Qn, preset, en, reset
  D_Flip_Flop #(.trigger("high")) d_ff_2 (.clk(and_1_out), .D(SL1), .Q(d_ff_2_q));  // open: Qn, preset, en, reset
  D_Flip_Flop #(.trigger("high")) d_ff_3 (.clk(and_1_out), .D(SL2), .Q(d_ff_3_q));  // open: Qn, preset, en, reset
  D_Flip_Flop #(.trigger("high")) d_ff_4 (.clk(and_1_out), .D(SL3), .Q(d_ff_4_q));  // open: Qn, preset, en, reset
  D_Flip_Flop #(.trigger("high")) d_ff_5 (.clk(and_1_out), .D(SL4), .Q(d_ff_5_q));  // open: Qn, preset, en, reset
  D_Flip_Flop #(.trigger("high")) d_ff_6 (.clk(and_1_out), .D(SL5), .Q(d_ff_6_q));  // open: Qn, preset, en, reset
  D_Flip_Flop #(.trigger("high")) d_ff_7 (.clk(and_1_out), .D(SL6), .Q(d_ff_7_q));  // open: Qn, preset, en, reset
  D_Flip_Flop #(.trigger("high")) d_ff_8 (.clk(and_1_out), .D(SL7), .Q(d_ff_8_q));  // open: Qn, preset, en, reset
  D_Flip_Flop #(.trigger("high")) d_ff_9 (.clk(ACLK), .D(d_ff_18_qn), .Qn(d_ff_9_qn));  // open: Q, preset, en, reset
  D_Flip_Flop #(.trigger("high")) d_ff_10 (.clk(ACLK), .D(d_ff_19_qn), .Qn(d_ff_10_qn));  // open: Q, preset, en, reset
  D_Flip_Flop #(.trigger("high")) d_ff_11 (.clk(ACLK), .D(d_ff_20_qn), .Qn(d_ff_11_qn));  // open: Q, preset, en, reset
  D_Flip_Flop #(.trigger("high")) d_ff_12 (.clk(ACLK), .D(d_ff_21_qn), .Qn(d_ff_12_qn));  // open: Q, preset, en, reset
  D_Flip_Flop #(.trigger("high")) d_ff_13 (.clk(ACLK), .D(d_ff_22_qn), .Qn(d_ff_13_qn));  // open: Q, preset, en, reset
  D_Flip_Flop #(.trigger("high")) d_ff_14 (.clk(ACLK), .D(d_ff_23_qn), .Qn(d_ff_14_qn));  // open: Q, preset, en, reset
  D_Flip_Flop #(.trigger("high")) d_ff_15 (.clk(ACLK), .D(d_ff_24_qn), .Qn(d_ff_15_qn));  // open: Q, preset, en, reset
  D_Flip_Flop #(.trigger("high")) d_ff_16 (.clk(ACLK), .D(1'b0), .Qn(d_ff_16_qn));  // open: Q, preset, en, reset
  and and_1 (and_1_out, PCM, nACLK);
  assign controlled_buffer_1_out = 1'b0 ? d_ff_9_qn : 1'bz;  // Controlled_Buffer controlled_buffer_1
  assign controlled_buffer_1_out = BLOAD ? d_ff_1_q : 1'bz;  // Controlled_Buffer controlled_buffer_2
  assign controlled_buffer_3_out = 1'b0 ? d_ff_10_qn : 1'bz;  // Controlled_Buffer controlled_buffer_3
  assign controlled_buffer_3_out = BLOAD ? d_ff_2_q : 1'bz;  // Controlled_Buffer controlled_buffer_4
  assign controlled_buffer_5_out = 1'b0 ? d_ff_11_qn : 1'bz;  // Controlled_Buffer controlled_buffer_5
  assign controlled_buffer_5_out = BLOAD ? d_ff_3_q : 1'bz;  // Controlled_Buffer controlled_buffer_6
  assign controlled_buffer_7_out = 1'b0 ? d_ff_12_qn : 1'bz;  // Controlled_Buffer controlled_buffer_7
  assign controlled_buffer_7_out = BLOAD ? d_ff_4_q : 1'bz;  // Controlled_Buffer controlled_buffer_8
  assign controlled_buffer_9_out = 1'b0 ? d_ff_13_qn : 1'bz;  // Controlled_Buffer controlled_buffer_9
  assign controlled_buffer_9_out = BLOAD ? d_ff_5_q : 1'bz;  // Controlled_Buffer controlled_buffer_10
  assign controlled_buffer_11_out = 1'b0 ? d_ff_14_qn : 1'bz;  // Controlled_Buffer controlled_buffer_11
  assign controlled_buffer_11_out = BLOAD ? d_ff_6_q : 1'bz;  // Controlled_Buffer controlled_buffer_12
  assign controlled_buffer_13_out = 1'b0 ? d_ff_15_qn : 1'bz;  // Controlled_Buffer controlled_buffer_13
  assign controlled_buffer_13_out = BLOAD ? d_ff_7_q : 1'bz;  // Controlled_Buffer controlled_buffer_14
  assign controlled_buffer_15_out = 1'b0 ? d_ff_16_qn : 1'bz;  // Controlled_Buffer controlled_buffer_15
  assign controlled_buffer_15_out = BLOAD ? d_ff_8_q : 1'bz;  // Controlled_Buffer controlled_buffer_16
  D_Flip_Flop #(.trigger("high")) d_ff_17 (
    .clk(nACLK), .D(controlled_buffer_1_out), .Q(BOUT), .reset(res));  // open: Qn, preset, en
  D_Flip_Flop #(.trigger("high")) d_ff_18 (
    .clk(nACLK), .D(controlled_buffer_3_out), .Qn(d_ff_18_qn), .reset(res));  // open: Q, preset, en
  D_Flip_Flop #(.trigger("high")) d_ff_19 (
    .clk(nACLK), .D(controlled_buffer_5_out), .Qn(d_ff_19_qn), .reset(res));  // open: Q, preset, en
  D_Flip_Flop #(.trigger("high")) d_ff_20 (
    .clk(nACLK), .D(controlled_buffer_7_out), .Qn(d_ff_20_qn), .reset(res));  // open: Q, preset, en
  D_Flip_Flop #(.trigger("high")) d_ff_21 (
    .clk(nACLK), .D(controlled_buffer_9_out), .Qn(d_ff_21_qn), .reset(res));  // open: Q, preset, en
  D_Flip_Flop #(.trigger("high")) d_ff_22 (
    .clk(nACLK), .D(controlled_buffer_11_out), .Qn(d_ff_22_qn), .reset(res));  // open: Q, preset, en
  D_Flip_Flop #(.trigger("high")) d_ff_23 (
    .clk(nACLK), .D(controlled_buffer_13_out), .Qn(d_ff_23_qn), .reset(res));  // open: Q, preset, en
  D_Flip_Flop #(.trigger("high")) d_ff_24 (
    .clk(nACLK), .D(controlled_buffer_15_out), .Qn(d_ff_24_qn), .reset(res));  // open: Q, preset, en
endmodule

module Register (
  input  ACLK,
  input  W40xx,
  input  D0,
  input  D1,
  input  D2,
  input  D3,
  input  D4,
  input  D5,
  input  D6,
  input  D7,
  output D0_2,
  output D1_2,
  output D2_2,
  output D3_2,
  output D4_2,
  output D5_2,
  output D6_2,
  output D7_2,
  output nD7
);

  wire and_1_out;

  and and_1 (and_1_out, ACLK, W40xx);
  Dlatch dlatch_1 (.EN(and_1_out), .IN(D0), .Q(D0_2));  // open: nQ
  Dlatch dlatch_2 (.EN(and_1_out), .IN(D1), .Q(D1_2));  // open: nQ
  Dlatch dlatch_3 (.EN(and_1_out), .IN(D2), .Q(D2_2));  // open: nQ
  Dlatch dlatch_4 (.EN(and_1_out), .IN(D3), .Q(D3_2));  // open: nQ
  Dlatch dlatch_5 (.EN(and_1_out), .IN(D4), .Q(D4_2));  // open: nQ
  Dlatch dlatch_6 (.EN(and_1_out), .IN(D5), .Q(D5_2));  // open: nQ
  Dlatch dlatch_7 (.EN(and_1_out), .IN(D6), .Q(D6_2));  // open: nQ
  Dlatch dlatch_8 (.EN(and_1_out), .IN(D7), .Q(D7_2), .nQ(nD7));
endmodule

module New_sample_shift_register (
  input  ACLK,
  input  nACLK,
  input  SL0,
  input  SL1,
  input  SL2,
  input  SL3,
  input  SL4,
  input  SL5,
  input  SL6,
  input  SL7,
  input  BSTEP,
  input  BLOAD,
  input  res,
  input  PCM,
  output BOUT
);

  wire and_1_out, and_2_out, and_3_out, and_4_out, and_5_out, and_6_out, and_7_out, and_8_out, and_9_out,
       and_10_out, and_11_out, and_12_out, and_13_out, and_14_out, and_15_out, and_16_out, d_ff_1_qn,
       d_ff_2_qn, d_ff_3_qn, d_ff_4_qn, d_ff_5_qn, d_ff_6_qn, d_ff_7_qn, d_ff_8_qn, d_ff_10_q, d_ff_11_q,
       d_ff_12_q, d_ff_13_q, d_ff_14_q, d_ff_15_q, d_ff_16_q, d_ff_17_q, d_ff_18_q, d_ff_19_q, d_ff_20_q,
       d_ff_21_q, d_ff_22_q, d_ff_23_q, not_1_out, not_2_out, not_3_out, not_4_out, not_5_out, not_6_out,
       not_7_out, not_8_out, or_1_out, or_2_out, or_3_out, or_4_out, or_5_out, or_6_out, or_7_out, or_8_out;

  D_Flip_Flop d_ff_1 (.clk(PCM), .D(SL0), .Qn(d_ff_1_qn));  // open: Q, preset, en, reset
  D_Flip_Flop d_ff_2 (.clk(PCM), .D(SL1), .Qn(d_ff_2_qn));  // open: Q, preset, en, reset
  D_Flip_Flop d_ff_3 (.clk(PCM), .D(SL2), .Qn(d_ff_3_qn));  // open: Q, preset, en, reset
  D_Flip_Flop d_ff_4 (.clk(PCM), .D(SL3), .Qn(d_ff_4_qn));  // open: Q, preset, en, reset
  D_Flip_Flop d_ff_5 (.clk(PCM), .D(SL4), .Qn(d_ff_5_qn));  // open: Q, preset, en, reset
  D_Flip_Flop d_ff_6 (.clk(PCM), .D(SL5), .Qn(d_ff_6_qn));  // open: Q, preset, en, reset
  D_Flip_Flop d_ff_7 (.clk(PCM), .D(SL6), .Qn(d_ff_7_qn));  // open: Q, preset, en, reset
  D_Flip_Flop d_ff_8 (.clk(PCM), .D(SL7), .Qn(d_ff_8_qn));  // open: Q, preset, en, reset
  and and_1 (and_1_out, BLOAD, d_ff_1_qn);
  and and_2 (and_2_out, BLOAD, not_1_out);
  not not_1 (not_1_out, d_ff_1_qn);
  and and_3 (and_3_out, BLOAD, d_ff_2_qn);
  and and_4 (and_4_out, BLOAD, not_2_out);
  not not_2 (not_2_out, d_ff_2_qn);
  and and_5 (and_5_out, BLOAD, d_ff_3_qn);
  and and_6 (and_6_out, BLOAD, not_3_out);
  not not_3 (not_3_out, d_ff_3_qn);
  and and_7 (and_7_out, BLOAD, d_ff_4_qn);
  and and_8 (and_8_out, BLOAD, not_4_out);
  not not_4 (not_4_out, d_ff_4_qn);
  and and_9 (and_9_out, BLOAD, d_ff_5_qn);
  and and_10 (and_10_out, BLOAD, not_5_out);
  not not_5 (not_5_out, d_ff_5_qn);
  and and_11 (and_11_out, BLOAD, d_ff_6_qn);
  and and_12 (and_12_out, BLOAD, not_6_out);
  not not_6 (not_6_out, d_ff_6_qn);
  and and_13 (and_13_out, BLOAD, d_ff_7_qn);
  and and_14 (and_14_out, BLOAD, not_7_out);
  not not_7 (not_7_out, d_ff_7_qn);
  and and_15 (and_15_out, BLOAD, d_ff_8_qn);
  and and_16 (and_16_out, BLOAD, not_8_out);
  not not_8 (not_8_out, d_ff_8_qn);
  D_Flip_Flop d_ff_9 (.clk(BSTEP), .D(d_ff_17_q), .Q(BOUT), .preset(or_1_out), .reset(and_2_out));  // open: Qn, en
  D_Flip_Flop d_ff_10 (
    .clk(BSTEP), .D(d_ff_18_q), .Q(d_ff_10_q), .preset(or_2_out), .reset(and_4_out));  // open: Qn, en
  D_Flip_Flop d_ff_11 (
    .clk(BSTEP), .D(d_ff_19_q), .Q(d_ff_11_q), .preset(or_3_out), .reset(and_6_out));  // open: Qn, en
  D_Flip_Flop d_ff_12 (
    .clk(BSTEP), .D(d_ff_20_q), .Q(d_ff_12_q), .preset(or_4_out), .reset(and_8_out));  // open: Qn, en
  D_Flip_Flop d_ff_13 (
    .clk(BSTEP), .D(d_ff_21_q), .Q(d_ff_13_q), .preset(or_5_out), .reset(and_10_out));  // open: Qn, en
  D_Flip_Flop d_ff_14 (
    .clk(BSTEP), .D(d_ff_22_q), .Q(d_ff_14_q), .preset(or_6_out), .reset(and_12_out));  // open: Qn, en
  D_Flip_Flop d_ff_15 (
    .clk(BSTEP), .D(d_ff_23_q), .Q(d_ff_15_q), .preset(or_7_out), .reset(and_14_out));  // open: Qn, en
  D_Flip_Flop d_ff_16 (.D(1'b0), .Q(d_ff_16_q), .preset(or_8_out), .en(1'b0), .reset(and_16_out));  // open: clk, Qn
  or or_1 (or_1_out, and_1_out, res);
  or or_2 (or_2_out, and_3_out, res);
  or or_3 (or_3_out, and_5_out, res);
  or or_4 (or_4_out, and_7_out, res);
  or or_5 (or_5_out, and_9_out, res);
  or or_6 (or_6_out, and_11_out, res);
  or or_7 (or_7_out, and_13_out, res);
  or or_8 (or_8_out, and_15_out, res);
  D_Flip_Flop d_ff_17 (.clk(nACLK), .D(d_ff_10_q), .Q(d_ff_17_q));  // open: Qn, preset, en, reset
  D_Flip_Flop d_ff_18 (.clk(nACLK), .D(d_ff_11_q), .Q(d_ff_18_q));  // open: Qn, preset, en, reset
  D_Flip_Flop d_ff_19 (.clk(nACLK), .D(d_ff_12_q), .Q(d_ff_19_q));  // open: Qn, preset, en, reset
  D_Flip_Flop d_ff_20 (.clk(nACLK), .D(d_ff_13_q), .Q(d_ff_20_q));  // open: Qn, preset, en, reset
  D_Flip_Flop d_ff_21 (.clk(nACLK), .D(d_ff_14_q), .Q(d_ff_21_q));  // open: Qn, preset, en, reset
  D_Flip_Flop d_ff_22 (.clk(nACLK), .D(d_ff_15_q), .Q(d_ff_22_q));  // open: Qn, preset, en, reset
  D_Flip_Flop d_ff_23 (.clk(nACLK), .D(d_ff_16_q), .Q(d_ff_23_q));  // open: Qn, preset, en, reset

  // Notes on the sheet:
  //   SL7 shift register bit connect clock to PHI2 data and enable to ground
  //   Buffer register connect clock to PHI1, enable to PCM
  //   Connect shift registers clock to PHI2, en signal to BSTEP, use latches connected between chains (clock /ACLK)
endmodule

module New_dmc_output_counter (
  input  nACLK,
  input  ACLK,
  input  W4011,
  input  DSTEP,
  input  RES,
  input  BOUT,
  input  DL0,
  input  DL1,
  input  DL2,
  input  DL3,
  input  DL4,
  input  DL5,
  input  DL6,
  output DMC0,
  output DMC1,
  output DMC2,
  output DMC3,
  output DMC4,
  output DMC5,
  output DMC6,
  output DOUT
);

  wire and_1_out, and_2_out, and_3_out, and_4_out, and_5_out, and_6_out, and_7_out, and_8_out, and_9_out,
       and_10_out, and_11_out, and_12_out, and_13_out, and_14_out, d_ff_2_qn, d_ff_3_qn, d_ff_4_qn,
       d_ff_5_qn, d_ff_6_qn, d_ff_7_qn, d_ff_8_q, d_ff_9_q, d_ff_10_q, d_ff_11_q, d_ff_12_q, d_ff_13_q,
       multiplexer_1_out, multiplexer_2_out, multiplexer_3_out, multiplexer_4_out, multiplexer_5_out,
       multiplexer_6_out, multiplexer_7_out, multiplexer_8_out, multiplexer_9_out, multiplexer_10_out,
       multiplexer_11_out, multiplexer_12_out, nor_1_out, nor_2_out, nor_3_out, nor_4_out, nor_5_out,
       not_1_out, not_2_out, not_3_out, not_4_out, not_5_out, not_6_out, not_7_out, not_8_out, not_9_out,
       not_10_out, not_11_out, not_12_out, or_1_out, or_2_out, or_3_out, or_4_out, or_5_out, or_6_out;

  and and_1 (and_1_out, ACLK, W4011);
  not not_1 (not_1_out, DL1);
  not not_2 (not_2_out, DL2);
  not not_3 (not_3_out, DL3);
  not not_4 (not_4_out, DL4);
  not not_5 (not_5_out, DL5);
  not not_6 (not_6_out, DL6);
  and and_2 (and_2_out, W4011, ACLK);
  and and_3 (and_3_out, DL1, and_1_out);
  and and_4 (and_4_out, not_1_out, and_1_out);
  and and_5 (and_5_out, DL2, and_1_out);
  and and_6 (and_6_out, not_2_out, and_1_out);
  and and_7 (and_7_out, DL3, and_1_out);
  and and_8 (and_8_out, not_3_out, and_1_out);
  and and_9 (and_9_out, DL4, and_1_out);
  and and_10 (and_10_out, not_4_out, and_1_out);
  and and_11 (and_11_out, DL5, and_1_out);
  and and_12 (and_12_out, not_5_out, and_1_out);
  and and_13 (and_13_out, DL6, and_1_out);
  and and_14 (and_14_out, not_6_out, and_1_out);
  D_Flip_Flop #(.trigger("high")) d_ff_1 (.clk(and_2_out), .D(DL0), .Q(DMC0));  // open: Qn, preset, en, reset
  D_Flip_Flop d_ff_2 (
    .clk(DSTEP), .D(d_ff_8_q), .Q(DMC1), .Qn(d_ff_2_qn), .preset(and_3_out), .reset(or_1_out));  // open: en
  or or_1 (or_1_out, RES, and_4_out);
  D_Flip_Flop d_ff_3 (
    .clk(DSTEP), .D(d_ff_9_q), .Q(DMC2), .Qn(d_ff_3_qn), .preset(and_5_out), .reset(or_2_out));  // open: en
  or or_2 (or_2_out, RES, and_6_out);
  D_Flip_Flop d_ff_4 (
    .clk(DSTEP), .D(d_ff_10_q), .Q(DMC3), .Qn(d_ff_4_qn), .preset(and_7_out), .reset(or_3_out));  // open: en
  or or_3 (or_3_out, RES, and_8_out);
  D_Flip_Flop d_ff_5 (
    .clk(DSTEP), .D(d_ff_11_q), .Q(DMC4), .Qn(d_ff_5_qn), .preset(and_9_out), .reset(or_4_out));  // open: en
  or or_4 (or_4_out, RES, and_10_out);
  D_Flip_Flop d_ff_6 (
    .clk(DSTEP), .D(d_ff_12_q), .Q(DMC5), .Qn(d_ff_6_qn), .preset(and_11_out), .reset(or_5_out));  // open: en
  or or_5 (or_5_out, RES, and_12_out);
  D_Flip_Flop d_ff_7 (
    .clk(DSTEP), .D(d_ff_13_q), .Q(DMC6), .Qn(d_ff_7_qn), .preset(and_13_out), .reset(or_6_out));  // open: en
  or or_6 (or_6_out, RES, and_14_out);
  Multiplexer multiplexer_1 (.in0(DMC1), .in1(d_ff_2_qn), .out(multiplexer_1_out), .sel(1'b1));  // open: en
  not not_7 (not_7_out, 1'b1);
  Multiplexer multiplexer_2 (.in0(DMC2), .in1(d_ff_3_qn), .out(multiplexer_2_out), .sel(nor_1_out));  // open: en
  not not_8 (not_8_out, nor_1_out);
  Multiplexer multiplexer_3 (.in0(DMC3), .in1(d_ff_4_qn), .out(multiplexer_3_out), .sel(nor_2_out));  // open: en
  not not_9 (not_9_out, nor_2_out);
  Multiplexer multiplexer_4 (.in0(DMC4), .in1(d_ff_5_qn), .out(multiplexer_4_out), .sel(nor_3_out));  // open: en
  not not_10 (not_10_out, nor_3_out);
  Multiplexer multiplexer_5 (.in0(DMC5), .in1(d_ff_6_qn), .out(multiplexer_5_out), .sel(nor_4_out));  // open: en
  not not_11 (not_11_out, nor_4_out);
  Multiplexer multiplexer_6 (.in0(DMC6), .in1(d_ff_7_qn), .out(multiplexer_6_out), .sel(nor_5_out));  // open: en
  not not_12 (not_12_out, nor_5_out);
  Multiplexer multiplexer_7 (.in0(d_ff_2_qn), .in1(DMC1), .out(multiplexer_7_out), .sel(BOUT));  // open: en
  Multiplexer multiplexer_8 (.in0(d_ff_3_qn), .in1(DMC2), .out(multiplexer_8_out), .sel(BOUT));  // open: en
  Multiplexer multiplexer_9 (.in0(d_ff_4_qn), .in1(DMC3), .out(multiplexer_9_out), .sel(BOUT));  // open: en
  Multiplexer multiplexer_10 (.in0(d_ff_5_qn), .in1(DMC4), .out(multiplexer_10_out), .sel(BOUT));  // open: en
  Multiplexer multiplexer_11 (.in0(d_ff_6_qn), .in1(DMC5), .out(multiplexer_11_out), .sel(BOUT));  // open: en
  Multiplexer multiplexer_12 (.in0(d_ff_7_qn), .in1(DMC6), .out(multiplexer_12_out), .sel(BOUT));  // open: en
  nor nor_1 (nor_1_out, multiplexer_7_out, not_7_out);
  nor nor_2 (nor_2_out, multiplexer_8_out, not_8_out);
  nor nor_3 (nor_3_out, multiplexer_9_out, not_9_out);
  nor nor_4 (nor_4_out, multiplexer_10_out, not_10_out);
  nor nor_5 (nor_5_out, multiplexer_11_out, not_11_out);
  nor nor_6 (DOUT, multiplexer_12_out, not_12_out);
  D_Flip_Flop d_ff_8 (.clk(nACLK), .D(multiplexer_1_out), .Q(d_ff_8_q));  // open: Qn, preset, en, reset
  D_Flip_Flop d_ff_9 (.clk(nACLK), .D(multiplexer_2_out), .Q(d_ff_9_q));  // open: Qn, preset, en, reset
  D_Flip_Flop d_ff_10 (.clk(nACLK), .D(multiplexer_3_out), .Q(d_ff_10_q));  // open: Qn, preset, en, reset
  D_Flip_Flop d_ff_11 (.clk(nACLK), .D(multiplexer_4_out), .Q(d_ff_11_q));  // open: Qn, preset, en, reset
  D_Flip_Flop d_ff_12 (.clk(nACLK), .D(multiplexer_5_out), .Q(d_ff_12_q));  // open: Qn, preset, en, reset
  D_Flip_Flop d_ff_13 (.clk(nACLK), .D(multiplexer_6_out), .Q(d_ff_13_q));  // open: Qn, preset, en, reset
  // Probe on {DMC6, DMC5, DMC4, DMC3, DMC2, DMC1}
endmodule

module Master_clock (
  input  PHI0,
  input  RES,
  output PHI1,
  output PHI2,
  output ACLK,
  output nACLK
);

  wire d_ff_1_qn, d_ff_2_qn, nor_1_out, nor_2_out, not_2_out;

  not not_1 (PHI1, PHI0);
  not not_2 (not_2_out, PHI1);
  D_Flip_Flop d_ff_1 (.clk(PHI1), .D(nor_1_out), .Qn(d_ff_1_qn));  // open: Q, preset, en, reset
  D_Flip_Flop d_ff_2 (.clk(PHI0), .D(d_ff_1_qn), .Qn(d_ff_2_qn));  // open: Q, preset, en, reset
  nor nor_1 (nor_1_out, d_ff_2_qn, RES);
  nor nor_2 (nor_2_out, nor_1_out, not_2_out);
  nor nor_3 (nACLK, not_2_out, PHI0, d_ff_2_qn);
  not not_3 (ACLK, nor_2_out);

  assign PHI2 = PHI0;

  // Notes on the sheet:
  //   INV1
  //   DL1
  //   DL2
  //   NOR1
  //   NOR2
  //   NOR3
endmodule
