// Logisim project iocontrol.circ as structural Verilog: 2 circuits, main circuit main
module main (
  input  in_1,
  input  W4016,
  input  D0,
  input  D1,
  input  D2,
  input  nRES_PIN,
  input  R_W_int,
  input  nR4016,
  input  nR4017,
  input  nNMI_PIN,
  input  nIRQ_PIN,
  input  INT_from_apu,
  input  CLK_PIN,
  output OUT0_PIN,
  output OUT1_PIN,
  output OUT2_PIN,
  output MASTER_RESET,
  output R_W_PIN,
  output IN0_PIN,
  output IN1_PIN,
  output nNMI_INT,
  output nIRQ_INT,
  output CLK_INT
);

  wire and_1_out, clock_1_out, d_ff_1_q, d_ff_2_q, d_ff_3_q, d_ff_4_q, d_ff_5_q, d_ff_6_q,
       masterclock_1_aclk, masterclock_1_phi2, not_1_out, not_3_out, not_4_out;

  Clock clock_1 (.out(clock_1_out));
  Masterclock masterclock_1 (
    .PHI0(clock_1_out), .RES(in_1), .PHI2(masterclock_1_phi2), .ACLK(masterclock_1_aclk));  // open: PHI1, nACLK
  not not_1 (not_1_out, masterclock_1_phi2);
  and and_1 (and_1_out, masterclock_1_aclk, W4016);
  not not_2 (nNMI_INT, not_3_out);
  D_Flip_Flop d_ff_1 (.clk(and_1_out), .D(D0), .Q(d_ff_1_q));  // open: Qn, preset, en, reset
  D_Flip_Flop d_ff_2 (.clk(and_1_out), .D(D1), .Q(d_ff_2_q));  // open: Qn, preset, en, reset
  D_Flip_Flop d_ff_3 (.clk(and_1_out), .D(D2), .Q(d_ff_3_q));  // open: Qn, preset, en, reset
  nor nor_1 (nIRQ_INT, not_4_out, INT_from_apu);
  D_Flip_Flop d_ff_4 (.clk(not_1_out), .D(d_ff_1_q), .Q(d_ff_4_q));  // open: Qn, preset, en, reset
  D_Flip_Flop d_ff_5 (.clk(not_1_out), .D(d_ff_2_q), .Q(d_ff_5_q));  // open: Qn, preset, en, reset
  D_Flip_Flop d_ff_6 (.clk(not_1_out), .D(d_ff_3_q), .Q(d_ff_6_q));  // open: Qn, preset, en, reset
  not not_3 (not_3_out, nNMI_PIN);
  not not_4 (not_4_out, nIRQ_PIN);
  assign OUT0_PIN = nRES_PIN ? d_ff_4_q : 1'bz;  // Controlled_Buffer controlled_buffer_1
  assign OUT1_PIN = nRES_PIN ? d_ff_5_q : 1'bz;  // Controlled_Buffer controlled_buffer_2
  assign OUT2_PIN = nRES_PIN ? d_ff_6_q : 1'bz;  // Controlled_Buffer controlled_buffer_3
  not not_5 (MASTER_RESET, nRES_PIN);
  assign R_W_PIN = nRES_PIN ? R_W_int : 1'bz;  // Controlled_Buffer controlled_buffer_4
  assign IN0_PIN = nRES_PIN ? nR4016 : 1'bz;  // Controlled_Buffer controlled_buffer_5
  assign IN1_PIN = nRES_PIN ? nR4017 : 1'bz;  // Controlled_Buffer controlled_buffer_6

  assign CLK_INT = CLK_PIN;
endmodule

module Masterclock (
  input  PHI0,
  input  RES,
  output PHI1,
  output PHI2,
  output ACLK,
  output nACLK
);

  wire d_ff_1_qn, d_ff_2_qn, nor_1_out, nor_2_out, not_2_out;

  not not_1 (PHI1, PHI0);
  not not_2 (not_2_out, PHI1);
  D_Flip_Flop d_ff_1 (.clk(PHI1), .D(nor_1_out), .Qn(d_ff_1_qn));  // open: Q, preset, en, reset
  D_Flip_Flop d_ff_2 (.clk(PHI0), .D(d_ff_1_qn), .Qn(d_ff_2_qn));  // open: Q, preset, en, reset
  nor nor_1 (nor_1_out, d_ff_2_qn, RES);
  nor nor_2 (nor_2_out, nor_1_out, not_2_out);
  nor nor_3 (nACLK, not_2_out, PHI0, d_ff_2_qn);
  not not_3 (ACLK, nor_2_out);

  assign PHI2 = PHI0;

  // Notes on the sheet:
  //   INV1
  //   DL1
  //   DL2
  //   NOR1
  //   NOR2
  //   NOR3
endmodule
