// Logisim project lfof1f2selector.circ as structural Verilog: 2 circuits, main circuit main
module main (
  input  Carry_In,
  input  Carry_In_2,
  input  T4,
  input  Z1,
  output ACLK,
  output nACLK,
  output F2,
  output out_8,
  output out,
  output out_10,
  output F1
);

  wire CLK_out, dlatch_1_nout, dlatch_2_nout, not_1_out, not_2_out, not_3_out, pull_resistor_4_node,
       pull_resistor_5_node, transistor_5_out, transistor_12_out;

  Clock CLK (.out(CLK_out));
  not not_1 (not_1_out, CLK_out);
  DLATCH dlatch_1 (.EN(CLK_out), .in(1'b0), .nout(dlatch_1_nout));  // open: out
  DLATCH dlatch_2 (.EN(not_1_out), .in(dlatch_1_nout), .nout(dlatch_2_nout));  // open: out
  Pull_Resistor #(.pull(1)) pull_resistor_1 (.node(F2));
  Transistor #(.\type ("n"), .gate("br")) transistor_1 (.in(1'b0), .out(F2), .gate(pull_resistor_4_node));
  Transistor #(.\type ("n")) transistor_2 (.in(1'b0), .out(F2), .gate(ACLK));
  Pull_Resistor #(.pull(1)) pull_resistor_2 (.node(F1));
  Transistor #(.\type ("n"), .gate("br")) transistor_3 (.in(1'b0), .out(F1), .gate(transistor_5_out));
  Transistor #(.\type ("n")) transistor_4 (.in(1'b0), .out(F1), .gate(ACLK));
  Transistor #(.\type ("n")) transistor_5 (.in(1'b0), .out(transistor_5_out), .gate(Carry_In_2));
  Transistor #(.\type ("n")) transistor_6 (.in(1'b0), .out(transistor_5_out), .gate(T4));
  Pull_Resistor #(.pull(1)) pull_resistor_3 (.node(transistor_5_out));
  Transistor #(.\type ("n")) transistor_7 (.in(1'b0), .out(transistor_5_out), .gate(Z1));
  not not_2 (not_2_out, dlatch_2_nout);
  Pull_Resistor #(.pull(1)) pull_resistor_4 (.node(pull_resistor_4_node));
  Transistor #(.\type ("n")) transistor_8 (.in(1'b0), .out(pull_resistor_4_node), .gate(transistor_5_out));
  Multiplexer multiplexer_1 (.in0(1'b0), .in1(not_2_out), .out(nACLK), .sel(CLK_out));  // open: en
  not not_3 (not_3_out, CLK_out);
  Transistor #(.\type ("n")) transistor_9 (.in(Carry_In), .out(out), .gate(F2));
  Transistor #(.\type ("n")) transistor_10 (.in(pull_resistor_5_node), .out(out), .gate(F1));
  Pull_Resistor #(.pull(1)) pull_resistor_5 (.node(pull_resistor_5_node));
  Multiplexer multiplexer_2 (.in0(not_3_out), .in1(1'b0), .out(ACLK), .sel(1'b0));  // open: en
  Pull_Resistor #(.pull(1)) pull_resistor_6 (.node(out_10));
  Transistor #(.\type ("n")) transistor_11 (.in(1'b0), .out(out_10), .gate(out));
  Transistor #(.\type ("n")) transistor_12 (.in(out_10), .out(transistor_12_out), .gate(nACLK));
  Pull_Resistor #(.pull(1)) pull_resistor_7 (.node(out_8));
  Transistor #(.\type ("n")) transistor_13 (.in(1'b0), .out(out_8), .gate(transistor_12_out));

  // Notes on the sheet:
  //   PHI1
  //   PHI2
endmodule

module DLATCH (
  input  EN,
  input  in,
  output out,
  output nout
);

  D_Flip_Flop #(.trigger("high")) d_ff_1 (.clk(EN), .D(in), .Q(out), .Qn(nout));  // open: preset, en, reset
endmodule
