// Logisim project lforesetcircuit.circ as structural Verilog: 1 circuit, main circuit main
module main (
  input  in_1,
  output out_2
);

  wire clock_1_out, d_ff_1_q, nor_1_out, nor_2_out, nor_3_out, not_1_out;

  Clock clock_1 (.out(clock_1_out));
  not not_1 (not_1_out, clock_1_out);
  nor nor_1 (nor_1_out, nor_3_out, nor_2_out);
  nor nor_2 (nor_2_out, nor_1_out, in_1, in_1);
  D_Flip_Flop #(.trigger("high")) d_ff_1 (.clk(not_1_out), .D(nor_2_out), .Q(d_ff_1_q));  // open: Qn, preset, en, reset
  nor nor_3 (nor_3_out, clock_1_out, d_ff_1_q);
  D_Flip_Flop #(.trigger("high")) d_ff_2 (.clk(not_1_out), .D(nor_2_out), .Qn(out_2));  // open: Q, preset, en, reset
endmodule
