// Logisim project newinputregister.circ as structural Verilog: 1 circuit, main circuit main
module main (
  input  PHI2,
  input  W40xx,
  input  D0,
  input  D1,
  input  D2,
  input  D3,
  input  D4,
  input  D5,
  input  D6,
  input  D7,
  output OUT0,
  output OUT1,
  output OUT2,
  output OUT3,
  output OUT4,
  output OUT5,
  output OUT6,
  output OUT7
);

  D_Flip_Flop d_ff_1 (.clk(PHI2), .D(D0), .Q(OUT0), .en(W40xx));  // open: Qn, preset, reset
  D_Flip_Flop d_ff_2 (.clk(PHI2), .D(D1), .Q(OUT1), .en(W40xx));  // open: Qn, preset, reset
  D_Flip_Flop d_ff_3 (.clk(PHI2), .D(D2), .Q(OUT2), .en(W40xx));  // open: Qn, preset, reset
  D_Flip_Flop d_ff_4 (.clk(PHI2), .D(D3), .Q(OUT3), .en(W40xx));  // open: Qn, preset, reset
  D_Flip_Flop d_ff_5 (.clk(PHI2), .D(D4), .Q(OUT4), .en(W40xx));  // open: Qn, preset, reset
  D_Flip_Flop d_ff_6 (.clk(PHI2), .D(D5), .Q(OUT5), .en(W40xx));  // open: Qn, preset, reset
  D_Flip_Flop d_ff_7 (.clk(PHI2), .D(D6), .Q(OUT6), .en(W40xx));  // open: Qn, preset, reset
  D_Flip_Flop d_ff_8 (.clk(PHI2), .D(D7), .Q(OUT7), .en(W40xx));  // open: Qn, preset, reset

  // Notes on the sheet:
  //   In triangle channel use PHI1 for high speed divider
  //   Replace all clock signals in counters  (lfo step and etc) with PHI2, instead of clock input use enable to step counters, lfsr and shift register
endmodule
