// Logisim project registerdecoder.circ as structural Verilog: 3 circuits, main circuit main
module main (
  input  in_1,
  input  in_2,
  input  in_3,
  input  in_4,
  input  in_5,
  input  in_6,
  input  in_7,
  input  in_8,
  input  in_9,
  input  in_10,
  input  in_11,
  input  in_12,
  input  in_13,
  input  in_14,
  input  in_15,
  input  in_16,
  input  in_17,
  input  in_18,
  output out_19,
  output out_20,
  output out_21,
  output out_22,
  output out_23,
  output out_24,
  output out_25,
  output out_26,
  output out_27,
  output out_28,
  output out_29,
  output out_30,
  output out_31,
  output out_32,
  output out_33,
  output out_34,
  output out_35,
  output out_36,
  output out_37,
  output out_38,
  output out_39,
  output out_40,
  output out_41,
  output out_42,
  output out_43,
  output out_44,
  output out_45
);

  Decoder decoder_1 (
    .A15(in_1), .A14(in_2), .A13(in_3), .A12(in_4), .A11(in_5), .A10(in_6), .A09(in_7), .A08(in_8),
    .A07(in_9), .A06(in_10), .A05(in_11), .R_W(in_12), .nR_W(out_23), .R_W_2(out_34));
  Table table_1 (
    .nR4015(out_19), .W4002(out_20), .W4001(out_22), .W4005(out_25), .W4006(out_26), .W4008(out_28),
    .W400A(out_30), .W400B(out_31), .W400E(out_33), .W4013(out_36), .W4012(out_37), .W4010(out_39),
    .W4014(out_41), .PHI1(in_18), .nR_WREG(out_23), .A0(in_17), .A1(in_16), .A2(in_15), .A3(in_14),
    .A4(in_13), .R_WREG(out_34), .W4003(out_21), .W4007(out_24), .W4004(out_27), .W400C(out_29),
    .W4000(out_32), .W4015(out_35), .W4011(out_38), .W400F(out_40), .nR4017(out_42), .nR4016(out_43),
    .W4016(out_44), .W4017(out_45));

  // Notes on the sheet:
  //   Register $4009 $400D  unused
endmodule

module Decoder (
  input  A15,
  input  A14,
  input  A13,
  input  A12,
  input  A11,
  input  A10,
  input  A09,
  input  A08,
  input  A07,
  input  A06,
  input  A05,
  input  R_W,
  output nR_W,
  output R_W_2
);

  wire pull_resistor_1_node, pull_resistor_2_node, pull_resistor_3_node, pull_resistor_4_node;

  Pull_Resistor #(.pull(1)) pull_resistor_1 (.node(pull_resistor_1_node));
  Pull_Resistor #(.pull(1)) pull_resistor_2 (.node(pull_resistor_2_node));
  Transistor #(.\type ("n")) transistor_1 (.in(1'b0), .out(pull_resistor_1_node), .gate(A15));
  Transistor #(.\type ("n"), .gate("br")) transistor_2 (.in(1'b0), .out(pull_resistor_2_node), .gate(A15));
  Transistor #(.\type ("n"), .gate("br")) transistor_3 (
    .in(1'b0), .out(pull_resistor_2_node), .gate(pull_resistor_3_node));
  Pull_Resistor #(.pull(1)) pull_resistor_3 (.node(pull_resistor_3_node));
  Transistor #(.\type ("n")) transistor_4 (.in(1'b0), .out(pull_resistor_3_node), .gate(A14));
  Transistor #(.\type ("n")) transistor_5 (.in(1'b0), .out(pull_resistor_2_node), .gate(R_W));
  Transistor #(.\type ("n")) transistor_6 (.in(1'b0), .out(pull_resistor_1_node), .gate(pull_resistor_3_node));
  Transistor #(.\type ("n"), .gate("br")) transistor_7 (.in(1'b0), .out(pull_resistor_2_node), .gate(A13));
  Transistor #(.\type ("n")) transistor_8 (.in(1'b0), .out(pull_resistor_1_node), .gate(A13));
  Transistor #(.\type ("n"), .gate("br")) transistor_9 (.in(1'b0), .out(pull_resistor_2_node), .gate(A12));
  Transistor #(.\type ("n")) transistor_10 (.in(1'b0), .out(pull_resistor_1_node), .gate(A12));
  Transistor #(.\type ("n"), .gate("br")) transistor_11 (.in(1'b0), .out(pull_resistor_2_node), .gate(A11));
  Transistor #(.\type ("n")) transistor_12 (.in(1'b0), .out(pull_resistor_1_node), .gate(A11));
  Transistor #(.\type ("n")) transistor_13 (.in(1'b0), .out(pull_resistor_1_node), .gate(A10));
  Transistor #(.\type ("n"), .gate("br")) transistor_14 (.in(1'b0), .out(pull_resistor_2_node), .gate(A10));
  Transistor #(.\type ("n"), .gate("br")) transistor_15 (.in(1'b0), .out(pull_resistor_2_node), .gate(A09));
  Transistor #(.\type ("n")) transistor_16 (.in(1'b0), .out(pull_resistor_1_node), .gate(A09));
  Transistor #(.\type ("n"), .gate("br")) transistor_17 (.in(1'b0), .out(pull_resistor_2_node), .gate(A08));
  Transistor #(.\type ("n")) transistor_18 (.in(1'b0), .out(pull_resistor_1_node), .gate(A08));
  Transistor #(.\type ("n"), .gate("br")) transistor_19 (.in(1'b0), .out(pull_resistor_2_node), .gate(A07));
  Transistor #(.\type ("n")) transistor_20 (.in(1'b0), .out(pull_resistor_1_node), .gate(A07));
  Transistor #(.\type ("n"), .gate("br")) transistor_21 (.in(1'b0), .out(pull_resistor_2_node), .gate(A06));
  Transistor #(.\type ("n"), .gate("br")) transistor_22 (.in(1'b0), .out(pull_resistor_2_node), .gate(A05));
  Transistor #(.\type ("n")) transistor_23 (.in(1'b0), .out(pull_resistor_1_node), .gate(A06));
  Transistor #(.\type ("n")) transistor_24 (.in(1'b0), .out(pull_resistor_1_node), .gate(A05));
  Transistor #(.\type ("n")) transistor_25 (.in(1'b0), .out(pull_resistor_1_node), .gate(pull_resistor_4_node));
  Pull_Resistor #(.pull(1)) pull_resistor_4 (.node(pull_resistor_4_node));
  Transistor #(.\type ("n")) transistor_26 (.in(1'b0), .out(pull_resistor_4_node), .gate(R_W));
  Pull_Resistor #(.pull(1)) pull_resistor_5 (.node(nR_W));
  Transistor #(.\type ("n")) transistor_27 (.in(1'b0), .out(nR_W), .gate(pull_resistor_1_node));
  Pull_Resistor #(.pull(1)) pull_resistor_6 (.node(R_W_2));
  Transistor #(.\type ("n")) transistor_28 (.in(1'b0), .out(R_W_2), .gate(pull_resistor_2_node));
endmodule

module Table (
  input  PHI1,
  input  nR_WREG,
  input  A0,
  input  A1,
  input  A2,
  input  A3,
  input  A4,
  input  R_WREG,
  output W4003,
  output W4007,
  output W4004,
  output nR4015,
  output W400C,
  output W4002,
  output W4000,
  output W4001,
  output W4015,
  output W4005,
  output W4006,
  output W4011,
  output W4008,
  output W400F,
  output W400A,
  output nR4017,
  output W400B,
  output nR4016,
  output W400E,
  output W4013,
  output W4016,
  output W4012,
  output W4017,
  output W4010,
  output W4014
);

  wire not_1_out, not_2_out, not_3_out, not_4_out, not_5_out, pull_resistor_14_node, pull_resistor_16_node,
       pull_resistor_17_node, pull_resistor_18_node, pull_resistor_23_node, pull_resistor_25_node,
       pull_resistor_26_node, pull_resistor_27_node, pull_resistor_28_node, pull_resistor_29_node,
       pull_resistor_56_node, pull_resistor_58_node, pull_resistor_60_node, pull_resistor_62_node,
       pull_resistor_64_node, pull_resistor_66_node, pull_resistor_68_node, pull_resistor_70_node,
       pull_resistor_74_node, pull_resistor_76_node, transistor_27_out, transistor_31_out, transistor_32_out,
       transistor_33_out, transistor_34_out, transistor_36_out, transistor_38_out, transistor_39_out,
       transistor_40_out, transistor_42_out, transistor_43_out, transistor_44_out, transistor_45_out,
       transistor_46_out, transistor_47_out, transistor_48_out, transistor_49_out, transistor_51_out,
       transistor_52_out, transistor_53_out, transistor_54_out, transistor_55_out, transistor_56_out,
       transistor_57_out, transistor_58_out, transistor_59_out, transistor_60_out, transistor_62_out,
       transistor_63_out, transistor_64_out, transistor_65_out;

  Transistor #(.\type ("n")) transistor_1 (.in(1'b0), .out(W4002), .gate(PHI1));
  Transistor #(.\type ("n")) transistor_2 (.in(1'b0), .out(W4001), .gate(PHI1));
  Transistor #(.\type ("n")) transistor_3 (.in(1'b0), .out(W4005), .gate(PHI1));
  Transistor #(.\type ("n")) transistor_4 (.in(1'b0), .out(W4006), .gate(PHI1));
  Transistor #(.\type ("n")) transistor_5 (.in(1'b0), .out(W4008), .gate(PHI1));
  Transistor #(.\type ("n")) transistor_6 (.in(1'b0), .out(W400A), .gate(PHI1));
  Transistor #(.\type ("n")) transistor_7 (.in(1'b0), .out(W400B), .gate(PHI1));
  Transistor #(.\type ("n")) transistor_8 (.in(1'b0), .out(W400E), .gate(PHI1));
  Transistor #(.\type ("n")) transistor_9 (.in(1'b0), .out(W4013), .gate(PHI1));
  Transistor #(.\type ("n")) transistor_10 (.in(1'b0), .out(W4012), .gate(PHI1));
  Transistor #(.\type ("n")) transistor_11 (.in(1'b0), .out(W4010), .gate(PHI1));
  Transistor #(.\type ("n")) transistor_12 (.in(1'b0), .out(W4014), .gate(PHI1));
  Transistor #(.\type ("n")) transistor_13 (.in(1'b0), .out(W4002), .gate(pull_resistor_14_node));
  Pull_Resistor #(.pull(1)) pull_resistor_1 (.node(W4002));
  Transistor #(.\type ("n")) transistor_14 (.in(1'b0), .out(W4001), .gate(transistor_27_out));
  Pull_Resistor #(.pull(1)) pull_resistor_2 (.node(W4001));
  Transistor #(.\type ("n")) transistor_15 (.in(1'b0), .out(W4005), .gate(pull_resistor_16_node));
  Pull_Resistor #(.pull(1)) pull_resistor_3 (.node(W4005));
  Pull_Resistor #(.pull(1)) pull_resistor_4 (.node(W4006));
  Transistor #(.\type ("n")) transistor_16 (.in(1'b0), .out(W4006), .gate(pull_resistor_17_node));
  Pull_Resistor #(.pull(1)) pull_resistor_5 (.node(W4008));
  Transistor #(.\type ("n")) transistor_17 (.in(1'b0), .out(W4008), .gate(pull_resistor_18_node));
  Transistor #(.\type ("n")) transistor_18 (.in(1'b0), .out(W400A), .gate(transistor_31_out));
  Pull_Resistor #(.pull(1)) pull_resistor_6 (.node(W400A));
  Pull_Resistor #(.pull(1)) pull_resistor_7 (.node(W400B));
  Transistor #(.\type ("n")) transistor_19 (.in(1'b0), .out(W400B), .gate(transistor_32_out));
  Pull_Resistor #(.pull(1)) pull_resistor_8 (.node(W400E));
  Transistor #(.\type ("n")) transistor_20 (.in(1'b0), .out(W400E), .gate(transistor_33_out));
  Pull_Resistor #(.pull(1)) pull_resistor_9 (.node(W4013));
  Transistor #(.\type ("n")) transistor_21 (.in(1'b0), .out(W4013), .gate(transistor_34_out));
  Transistor #(.\type ("n")) transistor_22 (.in(1'b0), .out(W4012), .gate(pull_resistor_23_node));
  Pull_Resistor #(.pull(1)) pull_resistor_10 (.node(W4012));
  Transistor #(.\type ("n")) transistor_23 (.in(1'b0), .out(W4010), .gate(transistor_36_out));
  Pull_Resistor #(.pull(1)) pull_resistor_11 (.node(W4010));
  Pull_Resistor #(.pull(1)) pull_resistor_12 (.node(W4014));
  Transistor #(.\type ("n")) transistor_24 (.in(1'b0), .out(W4014), .gate(pull_resistor_25_node));
  Pull_Resistor #(.pull(1)) pull_resistor_13 (.node(nR4015));
  Transistor #(.\type ("n")) transistor_25 (.in(1'b0), .out(nR4015), .gate(transistor_38_out));
  Pull_Resistor #(.pull(1)) pull_resistor_14 (.node(pull_resistor_14_node));
  Transistor #(.\type ("n")) transistor_26 (.in(1'b0), .out(pull_resistor_14_node), .gate(transistor_53_out));
  Transistor #(.\type ("n")) transistor_27 (.in(1'b0), .out(transistor_27_out), .gate(transistor_44_out));
  Pull_Resistor #(.pull(1)) pull_resistor_15 (.node(transistor_27_out));
  Pull_Resistor #(.pull(1)) pull_resistor_16 (.node(pull_resistor_16_node));
  Transistor #(.\type ("n")) transistor_28 (.in(1'b0), .out(pull_resistor_16_node), .gate(transistor_45_out));
  Pull_Resistor #(.pull(1)) pull_resistor_17 (.node(pull_resistor_17_node));
  Transistor #(.\type ("n")) transistor_29 (.in(1'b0), .out(pull_resistor_17_node), .gate(transistor_56_out));
  Pull_Resistor #(.pull(1)) pull_resistor_18 (.node(pull_resistor_18_node));
  Transistor #(.\type ("n")) transistor_30 (.in(1'b0), .out(pull_resistor_18_node), .gate(transistor_58_out));
  Transistor #(.\type ("n")) transistor_31 (.in(1'b0), .out(transistor_31_out), .gate(transistor_59_out));
  Pull_Resistor #(.pull(1)) pull_resistor_19 (.node(transistor_31_out));
  Transistor #(.\type ("n")) transistor_32 (.in(1'b0), .out(transistor_32_out), .gate(transistor_48_out));
  Pull_Resistor #(.pull(1)) pull_resistor_20 (.node(transistor_32_out));
  Transistor #(.\type ("n")) transistor_33 (.in(1'b0), .out(transistor_33_out), .gate(transistor_60_out));
  Pull_Resistor #(.pull(1)) pull_resistor_21 (.node(transistor_33_out));
  Transistor #(.\type ("n")) transistor_34 (.in(1'b0), .out(transistor_34_out), .gate(transistor_51_out));
  Pull_Resistor #(.pull(1)) pull_resistor_22 (.node(transistor_34_out));
  Pull_Resistor #(.pull(1)) pull_resistor_23 (.node(pull_resistor_23_node));
  Transistor #(.\type ("n")) transistor_35 (.in(1'b0), .out(pull_resistor_23_node), .gate(transistor_62_out));
  Transistor #(.\type ("n")) transistor_36 (.in(1'b0), .out(transistor_36_out), .gate(transistor_64_out));
  Pull_Resistor #(.pull(1)) pull_resistor_24 (.node(transistor_36_out));
  Pull_Resistor #(.pull(1)) pull_resistor_25 (.node(pull_resistor_25_node));
  Transistor #(.\type ("n")) transistor_37 (.in(1'b0), .out(pull_resistor_25_node), .gate(transistor_65_out));
  Transistor #(.\type ("n"), .gate("br")) transistor_38 (.in(1'b0), .out(transistor_38_out), .gate(nR_WREG));
  Transistor #(.\type ("n"), .gate("br")) transistor_39 (.in(1'b0), .out(transistor_39_out), .gate(nR_WREG));
  Transistor #(.\type ("n"), .gate("br")) transistor_40 (.in(1'b0), .out(transistor_40_out), .gate(nR_WREG));
  not not_1 (not_1_out, A0);
  Transistor #(.\type ("n"), .gate("br")) transistor_41 (.in(1'b0), .out(transistor_38_out), .gate(not_1_out));
  Transistor #(.\type ("n"), .gate("br")) transistor_42 (.in(1'b0), .out(transistor_42_out), .gate(not_1_out));
  Transistor #(.\type ("n"), .gate("br")) transistor_43 (.in(1'b0), .out(transistor_43_out), .gate(not_1_out));
  Transistor #(.\type ("n"), .gate("br")) transistor_44 (.in(1'b0), .out(transistor_44_out), .gate(not_1_out));
  Transistor #(.\type ("n"), .gate("br")) transistor_45 (.in(1'b0), .out(transistor_45_out), .gate(not_1_out));
  Transistor #(.\type ("n"), .gate("br")) transistor_46 (.in(1'b0), .out(transistor_46_out), .gate(not_1_out));
  Transistor #(.\type ("n"), .gate("br")) transistor_47 (.in(1'b0), .out(transistor_47_out), .gate(not_1_out));
  Transistor #(.\type ("n"), .gate("br")) transistor_48 (.in(1'b0), .out(transistor_48_out), .gate(not_1_out));
  Transistor #(.\type ("n"), .gate("br")) transistor_49 (.in(1'b0), .out(transistor_49_out), .gate(not_1_out));
  Transistor #(.\type ("n"), .gate("br")) transistor_50 (.in(1'b0), .out(transistor_39_out), .gate(not_1_out));
  Transistor #(.\type ("n"), .gate("br")) transistor_51 (.in(1'b0), .out(transistor_51_out), .gate(not_1_out));
  Transistor #(.\type ("n"), .gate("br")) transistor_52 (.in(1'b0), .out(transistor_52_out), .gate(not_1_out));
  Transistor #(.\type ("n"), .gate("br")) transistor_53 (.in(1'b0), .out(transistor_53_out), .gate(A0));
  Transistor #(.\type ("n"), .gate("br")) transistor_54 (.in(1'b0), .out(transistor_54_out), .gate(A0));
  Transistor #(.\type ("n"), .gate("br")) transistor_55 (.in(1'b0), .out(transistor_55_out), .gate(A0));
  Transistor #(.\type ("n"), .gate("br")) transistor_56 (.in(1'b0), .out(transistor_56_out), .gate(A0));
  Transistor #(.\type ("n"), .gate("br")) transistor_57 (.in(1'b0), .out(transistor_57_out), .gate(A0));
  Transistor #(.\type ("n"), .gate("br")) transistor_58 (.in(1'b0), .out(transistor_58_out), .gate(A0));
  Transistor #(.\type ("n"), .gate("br")) transistor_59 (.in(1'b0), .out(transistor_59_out), .gate(A0));
  Transistor #(.\type ("n"), .gate("br")) transistor_60 (.in(1'b0), .out(transistor_60_out), .gate(A0));
  Transistor #(.\type ("n"), .gate("br")) transistor_61 (.in(1'b0), .out(transistor_40_out), .gate(A0));
  Transistor #(.\type ("n"), .gate("br")) transistor_62 (.in(1'b0), .out(transistor_62_out), .gate(A0));
  Transistor #(.\type ("n"), .gate("br")) transistor_63 (.in(1'b0), .out(transistor_63_out), .gate(A0));
  Transistor #(.\type ("n"), .gate("br")) transistor_64 (.in(1'b0), .out(transistor_64_out), .gate(A0));
  Transistor #(.\type ("n"), .gate("br")) transistor_65 (.in(1'b0), .out(transistor_65_out), .gate(A0));
  not not_2 (not_2_out, A1);
  Transistor #(.\type ("n"), .gate("br")) transistor_66 (.in(1'b0), .out(transistor_38_out), .gate(A1));
  Transistor #(.\type ("n"), .gate("br")) transistor_67 (.in(1'b0), .out(transistor_42_out), .gate(not_2_out));
  Transistor #(.\type ("n"), .gate("br")) transistor_68 (.in(1'b0), .out(transistor_53_out), .gate(not_2_out));
  Transistor #(.\type ("n"), .gate("br")) transistor_69 (.in(1'b0), .out(transistor_43_out), .gate(not_2_out));
  Transistor #(.\type ("n"), .gate("br")) transistor_70 (.in(1'b0), .out(transistor_44_out), .gate(A1));
  Transistor #(.\type ("n"), .gate("br")) transistor_71 (.in(1'b0), .out(transistor_54_out), .gate(A1));
  Transistor #(.\type ("n"), .gate("br")) transistor_72 (.in(1'b0), .out(transistor_45_out), .gate(A1));
  Transistor #(.\type ("n"), .gate("br")) transistor_73 (.in(1'b0), .out(transistor_55_out), .gate(A1));
  Transistor #(.\type ("n"), .gate("br")) transistor_74 (.in(1'b0), .out(transistor_56_out), .gate(not_2_out));
  Transistor #(.\type ("n"), .gate("br")) transistor_75 (.in(1'b0), .out(transistor_57_out), .gate(A1));
  Transistor #(.\type ("n"), .gate("br")) transistor_76 (.in(1'b0), .out(transistor_58_out), .gate(A1));
  Transistor #(.\type ("n"), .gate("br")) transistor_77 (.in(1'b0), .out(transistor_46_out), .gate(A1));
  Transistor #(.\type ("n"), .gate("br")) transistor_78 (.in(1'b0), .out(transistor_59_out), .gate(not_2_out));
  Transistor #(.\type ("n"), .gate("br")) transistor_79 (.in(1'b0), .out(transistor_47_out), .gate(A1));
  Transistor #(.\type ("n"), .gate("br")) transistor_80 (.in(1'b0), .out(transistor_48_out), .gate(not_2_out));
  Transistor #(.\type ("n"), .gate("br")) transistor_81 (.in(1'b0), .out(transistor_49_out), .gate(not_2_out));
  Transistor #(.\type ("n"), .gate("br")) transistor_82 (.in(1'b0), .out(transistor_60_out), .gate(not_2_out));
  Transistor #(.\type ("n"), .gate("br")) transistor_83 (.in(1'b0), .out(transistor_39_out), .gate(not_2_out));
  Transistor #(.\type ("n"), .gate("br")) transistor_84 (.in(1'b0), .out(transistor_51_out), .gate(not_2_out));
  Transistor #(.\type ("n"), .gate("br")) transistor_85 (.in(1'b0), .out(transistor_40_out), .gate(not_2_out));
  Transistor #(.\type ("n"), .gate("br")) transistor_86 (.in(1'b0), .out(transistor_62_out), .gate(not_2_out));
  Transistor #(.\type ("n"), .gate("br")) transistor_87 (.in(1'b0), .out(transistor_63_out), .gate(not_2_out));
  Transistor #(.\type ("n"), .gate("br")) transistor_88 (.in(1'b0), .out(transistor_64_out), .gate(A1));
  Transistor #(.\type ("n"), .gate("br")) transistor_89 (.in(1'b0), .out(transistor_52_out), .gate(not_2_out));
  Transistor #(.\type ("n"), .gate("br")) transistor_90 (.in(1'b0), .out(transistor_65_out), .gate(A1));
  Transistor #(.\type ("n"), .gate("br")) transistor_91 (.in(1'b0), .out(transistor_38_out), .gate(not_3_out));
  Transistor #(.\type ("n"), .gate("br")) transistor_92 (.in(1'b0), .out(transistor_43_out), .gate(not_3_out));
  Transistor #(.\type ("n"), .gate("br")) transistor_93 (.in(1'b0), .out(transistor_54_out), .gate(not_3_out));
  Transistor #(.\type ("n"), .gate("br")) transistor_94 (.in(1'b0), .out(transistor_45_out), .gate(not_3_out));
  Transistor #(.\type ("n"), .gate("br")) transistor_95 (.in(1'b0), .out(transistor_55_out), .gate(not_3_out));
  Transistor #(.\type ("n"), .gate("br")) transistor_96 (.in(1'b0), .out(transistor_56_out), .gate(not_3_out));
  Transistor #(.\type ("n"), .gate("br")) transistor_97 (.in(1'b0), .out(transistor_46_out), .gate(not_3_out));
  Transistor #(.\type ("n"), .gate("br")) transistor_98 (.in(1'b0), .out(transistor_49_out), .gate(not_3_out));
  Transistor #(.\type ("n"), .gate("br")) transistor_99 (.in(1'b0), .out(transistor_60_out), .gate(not_3_out));
  Transistor #(.\type ("n"), .gate("br")) transistor_100 (.in(1'b0), .out(transistor_39_out), .gate(not_3_out));
  Transistor #(.\type ("n"), .gate("br")) transistor_101 (.in(1'b0), .out(transistor_40_out), .gate(not_3_out));
  Transistor #(.\type ("n"), .gate("br")) transistor_102 (.in(1'b0), .out(transistor_63_out), .gate(not_3_out));
  Transistor #(.\type ("n"), .gate("br")) transistor_103 (.in(1'b0), .out(transistor_52_out), .gate(not_3_out));
  Transistor #(.\type ("n"), .gate("br")) transistor_104 (.in(1'b0), .out(transistor_65_out), .gate(not_3_out));
  not not_3 (not_3_out, A2);
  Transistor #(.\type ("n"), .gate("br")) transistor_105 (.in(1'b0), .out(transistor_42_out), .gate(A2));
  Transistor #(.\type ("n"), .gate("br")) transistor_106 (.in(1'b0), .out(transistor_53_out), .gate(A2));
  Transistor #(.\type ("n"), .gate("br")) transistor_107 (.in(1'b0), .out(transistor_44_out), .gate(A2));
  Transistor #(.\type ("n"), .gate("br")) transistor_108 (.in(1'b0), .out(transistor_57_out), .gate(A2));
  Transistor #(.\type ("n"), .gate("br")) transistor_109 (.in(1'b0), .out(transistor_58_out), .gate(A2));
  Transistor #(.\type ("n"), .gate("br")) transistor_110 (.in(1'b0), .out(transistor_59_out), .gate(A2));
  Transistor #(.\type ("n"), .gate("br")) transistor_111 (.in(1'b0), .out(transistor_47_out), .gate(A2));
  Transistor #(.\type ("n"), .gate("br")) transistor_112 (.in(1'b0), .out(transistor_48_out), .gate(A2));
  Transistor #(.\type ("n"), .gate("br")) transistor_113 (.in(1'b0), .out(transistor_51_out), .gate(A2));
  Transistor #(.\type ("n"), .gate("br")) transistor_114 (.in(1'b0), .out(transistor_62_out), .gate(A2));
  Transistor #(.\type ("n"), .gate("br")) transistor_115 (.in(1'b0), .out(transistor_64_out), .gate(A2));
  Transistor #(.\type ("n"), .gate("br")) transistor_116 (.in(1'b0), .out(transistor_55_out), .gate(not_4_out));
  Transistor #(.\type ("n"), .gate("br")) transistor_117 (.in(1'b0), .out(transistor_58_out), .gate(not_4_out));
  Transistor #(.\type ("n"), .gate("br")) transistor_118 (.in(1'b0), .out(transistor_59_out), .gate(not_4_out));
  Transistor #(.\type ("n"), .gate("br")) transistor_119 (.in(1'b0), .out(transistor_48_out), .gate(not_4_out));
  Transistor #(.\type ("n"), .gate("br")) transistor_120 (.in(1'b0), .out(transistor_49_out), .gate(not_4_out));
  Transistor #(.\type ("n"), .gate("br")) transistor_121 (.in(1'b0), .out(transistor_60_out), .gate(not_4_out));
  not not_4 (not_4_out, A3);
  Transistor #(.\type ("n"), .gate("br")) transistor_122 (.in(1'b0), .out(transistor_38_out), .gate(A3));
  Transistor #(.\type ("n"), .gate("br")) transistor_123 (.in(1'b0), .out(transistor_42_out), .gate(A3));
  Transistor #(.\type ("n"), .gate("br")) transistor_124 (.in(1'b0), .out(transistor_53_out), .gate(A3));
  Transistor #(.\type ("n"), .gate("br")) transistor_125 (.in(1'b0), .out(transistor_43_out), .gate(A3));
  Transistor #(.\type ("n"), .gate("br")) transistor_126 (.in(1'b0), .out(transistor_44_out), .gate(A3));
  Transistor #(.\type ("n"), .gate("br")) transistor_127 (.in(1'b0), .out(transistor_54_out), .gate(A3));
  Transistor #(.\type ("n"), .gate("br")) transistor_128 (.in(1'b0), .out(transistor_45_out), .gate(A3));
  Transistor #(.\type ("n"), .gate("br")) transistor_129 (.in(1'b0), .out(transistor_56_out), .gate(A3));
  Transistor #(.\type ("n"), .gate("br")) transistor_130 (.in(1'b0), .out(transistor_57_out), .gate(A3));
  Transistor #(.\type ("n"), .gate("br")) transistor_131 (.in(1'b0), .out(transistor_46_out), .gate(A3));
  Transistor #(.\type ("n"), .gate("br")) transistor_132 (.in(1'b0), .out(transistor_47_out), .gate(A3));
  Transistor #(.\type ("n"), .gate("br")) transistor_133 (.in(1'b0), .out(transistor_39_out), .gate(A3));
  Transistor #(.\type ("n"), .gate("br")) transistor_134 (.in(1'b0), .out(transistor_40_out), .gate(A3));
  Transistor #(.\type ("n"), .gate("br")) transistor_135 (.in(1'b0), .out(transistor_62_out), .gate(A3));
  Transistor #(.\type ("n"), .gate("br")) transistor_136 (.in(1'b0), .out(transistor_63_out), .gate(A3));
  Transistor #(.\type ("n"), .gate("br")) transistor_137 (.in(1'b0), .out(transistor_64_out), .gate(A3));
  Transistor #(.\type ("n"), .gate("br")) transistor_138 (.in(1'b0), .out(transistor_52_out), .gate(A3));
  Transistor #(.\type ("n"), .gate("br")) transistor_139 (.in(1'b0), .out(transistor_65_out), .gate(A3));
  not not_5 (not_5_out, A4);
  Transistor #(.\type ("n"), .gate("br")) transistor_140 (.in(1'b0), .out(transistor_38_out), .gate(not_5_out));
  Transistor #(.\type ("n"), .gate("br")) transistor_141 (.in(1'b0), .out(transistor_46_out), .gate(not_5_out));
  Transistor #(.\type ("n"), .gate("br")) transistor_142 (.in(1'b0), .out(transistor_47_out), .gate(not_5_out));
  Transistor #(.\type ("n"), .gate("br")) transistor_143 (.in(1'b0), .out(transistor_39_out), .gate(not_5_out));
  Transistor #(.\type ("n"), .gate("br")) transistor_144 (.in(1'b0), .out(transistor_51_out), .gate(not_5_out));
  Transistor #(.\type ("n"), .gate("br")) transistor_145 (.in(1'b0), .out(transistor_40_out), .gate(not_5_out));
  Transistor #(.\type ("n"), .gate("br")) transistor_146 (.in(1'b0), .out(transistor_62_out), .gate(not_5_out));
  Transistor #(.\type ("n"), .gate("br")) transistor_147 (.in(1'b0), .out(transistor_63_out), .gate(not_5_out));
  Transistor #(.\type ("n"), .gate("br")) transistor_148 (.in(1'b0), .out(transistor_64_out), .gate(not_5_out));
  Transistor #(.\type ("n"), .gate("br")) transistor_149 (.in(1'b0), .out(transistor_52_out), .gate(not_5_out));
  Transistor #(.\type ("n"), .gate("br")) transistor_150 (.in(1'b0), .out(transistor_65_out), .gate(not_5_out));
  Transistor #(.\type ("n"), .gate("br")) transistor_151 (.in(1'b0), .out(transistor_42_out), .gate(A4));
  Transistor #(.\type ("n"), .gate("br")) transistor_152 (.in(1'b0), .out(transistor_53_out), .gate(A4));
  Transistor #(.\type ("n"), .gate("br")) transistor_153 (.in(1'b0), .out(transistor_43_out), .gate(A4));
  Transistor #(.\type ("n"), .gate("br")) transistor_154 (.in(1'b0), .out(transistor_44_out), .gate(A4));
  Transistor #(.\type ("n"), .gate("br")) transistor_155 (.in(1'b0), .out(transistor_54_out), .gate(A4));
  Transistor #(.\type ("n"), .gate("br")) transistor_156 (.in(1'b0), .out(transistor_45_out), .gate(A4));
  Transistor #(.\type ("n"), .gate("br")) transistor_157 (.in(1'b0), .out(transistor_55_out), .gate(A4));
  Transistor #(.\type ("n"), .gate("br")) transistor_158 (.in(1'b0), .out(transistor_56_out), .gate(A4));
  Transistor #(.\type ("n"), .gate("br")) transistor_159 (.in(1'b0), .out(transistor_57_out), .gate(A4));
  Transistor #(.\type ("n"), .gate("br")) transistor_160 (.in(1'b0), .out(transistor_58_out), .gate(A4));
  Transistor #(.\type ("n"), .gate("br")) transistor_161 (.in(1'b0), .out(transistor_59_out), .gate(A4));
  Transistor #(.\type ("n"), .gate("br")) transistor_162 (.in(1'b0), .out(transistor_48_out), .gate(A4));
  Transistor #(.\type ("n"), .gate("br")) transistor_163 (.in(1'b0), .out(transistor_49_out), .gate(A4));
  Transistor #(.\type ("n"), .gate("br")) transistor_164 (.in(1'b0), .out(transistor_60_out), .gate(A4));
  Pull_Resistor #(.pull(1)) pull_resistor_26 (.node(pull_resistor_26_node));
  Pull_Resistor #(.pull(1)) pull_resistor_27 (.node(pull_resistor_27_node));
  Pull_Resistor #(.pull(1)) pull_resistor_28 (.node(pull_resistor_28_node));
  Pull_Resistor #(.pull(1)) pull_resistor_29 (.node(pull_resistor_29_node));
  Pull_Resistor #(.pull(1)) pull_resistor_30 (.node(transistor_38_out));
  Pull_Resistor #(.pull(1)) pull_resistor_31 (.node(transistor_42_out));
  Transistor #(.\type ("n"), .gate("br")) transistor_165 (.in(1'b0), .out(transistor_42_out), .gate(R_WREG));
  Transistor #(.\type ("n"), .gate("br")) transistor_166 (.in(1'b0), .out(transistor_53_out), .gate(R_WREG));
  Pull_Resistor #(.pull(1)) pull_resistor_32 (.node(transistor_53_out));
  Pull_Resistor #(.pull(1)) pull_resistor_33 (.node(transistor_43_out));
  Transistor #(.\type ("n"), .gate("br")) transistor_167 (.in(1'b0), .out(transistor_43_out), .gate(R_WREG));
  Pull_Resistor #(.pull(1)) pull_resistor_34 (.node(transistor_44_out));
  Transistor #(.\type ("n"), .gate("br")) transistor_168 (.in(1'b0), .out(transistor_44_out), .gate(R_WREG));
  Transistor #(.\type ("n"), .gate("br")) transistor_169 (.in(1'b0), .out(transistor_54_out), .gate(R_WREG));
  Pull_Resistor #(.pull(1)) pull_resistor_35 (.node(transistor_54_out));
  Transistor #(.\type ("n"), .gate("br")) transistor_170 (.in(1'b0), .out(transistor_45_out), .gate(R_WREG));
  Pull_Resistor #(.pull(1)) pull_resistor_36 (.node(transistor_45_out));
  Transistor #(.\type ("n"), .gate("br")) transistor_171 (.in(1'b0), .out(transistor_55_out), .gate(R_WREG));
  Pull_Resistor #(.pull(1)) pull_resistor_37 (.node(transistor_55_out));
  Pull_Resistor #(.pull(1)) pull_resistor_38 (.node(transistor_56_out));
  Transistor #(.\type ("n"), .gate("br")) transistor_172 (.in(1'b0), .out(transistor_56_out), .gate(R_WREG));
  Pull_Resistor #(.pull(1)) pull_resistor_39 (.node(transistor_57_out));
  Transistor #(.\type ("n"), .gate("br")) transistor_173 (.in(1'b0), .out(transistor_57_out), .gate(R_WREG));
  Transistor #(.\type ("n"), .gate("br")) transistor_174 (.in(1'b0), .out(transistor_58_out), .gate(R_WREG));
  Pull_Resistor #(.pull(1)) pull_resistor_40 (.node(transistor_58_out));
  Transistor #(.\type ("n"), .gate("br")) transistor_175 (.in(1'b0), .out(transistor_46_out), .gate(R_WREG));
  Pull_Resistor #(.pull(1)) pull_resistor_41 (.node(transistor_46_out));
  Pull_Resistor #(.pull(1)) pull_resistor_42 (.node(transistor_59_out));
  Transistor #(.\type ("n"), .gate("br")) transistor_176 (.in(1'b0), .out(transistor_59_out), .gate(R_WREG));
  Transistor #(.\type ("n"), .gate("br")) transistor_177 (.in(1'b0), .out(transistor_47_out), .gate(R_WREG));
  Pull_Resistor #(.pull(1)) pull_resistor_43 (.node(transistor_47_out));
  Pull_Resistor #(.pull(1)) pull_resistor_44 (.node(transistor_48_out));
  Transistor #(.\type ("n"), .gate("br")) transistor_178 (.in(1'b0), .out(transistor_48_out), .gate(R_WREG));
  Transistor #(.\type ("n"), .gate("br")) transistor_179 (.in(1'b0), .out(transistor_49_out), .gate(R_WREG));
  Pull_Resistor #(.pull(1)) pull_resistor_45 (.node(transistor_49_out));
  Transistor #(.\type ("n"), .gate("br")) transistor_180 (.in(1'b0), .out(transistor_60_out), .gate(R_WREG));
  Pull_Resistor #(.pull(1)) pull_resistor_46 (.node(transistor_60_out));
  Pull_Resistor #(.pull(1)) pull_resistor_47 (.node(transistor_39_out));
  Pull_Resistor #(.pull(1)) pull_resistor_48 (.node(transistor_51_out));
  Transistor #(.\type ("n"), .gate("br")) transistor_181 (.in(1'b0), .out(transistor_51_out), .gate(R_WREG));
  Pull_Resistor #(.pull(1)) pull_resistor_49 (.node(transistor_40_out));
  Transistor #(.\type ("n"), .gate("br")) transistor_182 (.in(1'b0), .out(transistor_62_out), .gate(R_WREG));
  Pull_Resistor #(.pull(1)) pull_resistor_50 (.node(transistor_62_out));
  Pull_Resistor #(.pull(1)) pull_resistor_51 (.node(transistor_63_out));
  Transistor #(.\type ("n"), .gate("br")) transistor_183 (.in(1'b0), .out(transistor_63_out), .gate(R_WREG));
  Pull_Resistor #(.pull(1)) pull_resistor_52 (.node(transistor_64_out));
  Transistor #(.\type ("n"), .gate("br")) transistor_184 (.in(1'b0), .out(transistor_64_out), .gate(R_WREG));
  Pull_Resistor #(.pull(1)) pull_resistor_53 (.node(transistor_52_out));
  Transistor #(.\type ("n"), .gate("br")) transistor_185 (.in(1'b0), .out(transistor_52_out), .gate(R_WREG));
  Transistor #(.\type ("n"), .gate("br")) transistor_186 (.in(1'b0), .out(transistor_65_out), .gate(R_WREG));
  Pull_Resistor #(.pull(1)) pull_resistor_54 (.node(transistor_65_out));
  Pull_Resistor #(.pull(1)) pull_resistor_55 (.node(W4003));
  Transistor #(.\type ("n")) transistor_187 (.in(1'b0), .out(W4003), .gate(pull_resistor_56_node));
  Pull_Resistor #(.pull(1)) pull_resistor_56 (.node(pull_resistor_56_node));
  Transistor #(.\type ("n")) transistor_188 (.in(1'b0), .out(pull_resistor_56_node), .gate(transistor_42_out));
  Pull_Resistor #(.pull(1)) pull_resistor_57 (.node(W4007));
  Transistor #(.\type ("n")) transistor_189 (.in(1'b0), .out(W4007), .gate(pull_resistor_58_node));
  Pull_Resistor #(.pull(1)) pull_resistor_58 (.node(pull_resistor_58_node));
  Transistor #(.\type ("n")) transistor_190 (.in(1'b0), .out(pull_resistor_58_node), .gate(transistor_43_out));
  Pull_Resistor #(.pull(1)) pull_resistor_59 (.node(W4004));
  Transistor #(.\type ("n")) transistor_191 (.in(1'b0), .out(W4004), .gate(pull_resistor_60_node));
  Pull_Resistor #(.pull(1)) pull_resistor_60 (.node(pull_resistor_60_node));
  Transistor #(.\type ("n")) transistor_192 (.in(1'b0), .out(pull_resistor_60_node), .gate(transistor_54_out));
  Pull_Resistor #(.pull(1)) pull_resistor_61 (.node(W400C));
  Transistor #(.\type ("n")) transistor_193 (.in(1'b0), .out(W400C), .gate(pull_resistor_62_node));
  Pull_Resistor #(.pull(1)) pull_resistor_62 (.node(pull_resistor_62_node));
  Transistor #(.\type ("n")) transistor_194 (.in(1'b0), .out(pull_resistor_62_node), .gate(transistor_55_out));
  Pull_Resistor #(.pull(1)) pull_resistor_63 (.node(W4000));
  Transistor #(.\type ("n")) transistor_195 (.in(1'b0), .out(W4000), .gate(pull_resistor_64_node));
  Pull_Resistor #(.pull(1)) pull_resistor_64 (.node(pull_resistor_64_node));
  Transistor #(.\type ("n")) transistor_196 (.in(1'b0), .out(pull_resistor_64_node), .gate(transistor_57_out));
  Pull_Resistor #(.pull(1)) pull_resistor_65 (.node(W4015));
  Transistor #(.\type ("n")) transistor_197 (.in(1'b0), .out(W4015), .gate(pull_resistor_66_node));
  Pull_Resistor #(.pull(1)) pull_resistor_66 (.node(pull_resistor_66_node));
  Transistor #(.\type ("n")) transistor_198 (.in(1'b0), .out(pull_resistor_66_node), .gate(transistor_46_out));
  Pull_Resistor #(.pull(1)) pull_resistor_67 (.node(W4011));
  Transistor #(.\type ("n")) transistor_199 (.in(1'b0), .out(W4011), .gate(pull_resistor_68_node));
  Pull_Resistor #(.pull(1)) pull_resistor_68 (.node(pull_resistor_68_node));
  Transistor #(.\type ("n")) transistor_200 (.in(1'b0), .out(pull_resistor_68_node), .gate(transistor_47_out));
  Pull_Resistor #(.pull(1)) pull_resistor_69 (.node(W400F));
  Transistor #(.\type ("n")) transistor_201 (.in(1'b0), .out(W400F), .gate(pull_resistor_70_node));
  Pull_Resistor #(.pull(1)) pull_resistor_70 (.node(pull_resistor_70_node));
  Transistor #(.\type ("n")) transistor_202 (.in(1'b0), .out(pull_resistor_70_node), .gate(transistor_49_out));
  Pull_Resistor #(.pull(1)) pull_resistor_71 (.node(nR4017));
  Transistor #(.\type ("n")) transistor_203 (.in(1'b0), .out(nR4017), .gate(transistor_39_out));
  Pull_Resistor #(.pull(1)) pull_resistor_72 (.node(nR4016));
  Transistor #(.\type ("n")) transistor_204 (.in(1'b0), .out(nR4016), .gate(transistor_40_out));
  Pull_Resistor #(.pull(1)) pull_resistor_73 (.node(W4016));
  Transistor #(.\type ("n")) transistor_205 (.in(1'b0), .out(W4016), .gate(pull_resistor_74_node));
  Pull_Resistor #(.pull(1)) pull_resistor_74 (.node(pull_resistor_74_node));
  Transistor #(.\type ("n")) transistor_206 (.in(1'b0), .out(pull_resistor_74_node), .gate(transistor_63_out));
  Pull_Resistor #(.pull(1)) pull_resistor_75 (.node(W4017));
  Transistor #(.\type ("n")) transistor_207 (.in(1'b0), .out(W4017), .gate(pull_resistor_76_node));
  Pull_Resistor #(.pull(1)) pull_resistor_76 (.node(pull_resistor_76_node));
  Transistor #(.\type ("n")) transistor_208 (.in(1'b0), .out(pull_resistor_76_node), .gate(transistor_52_out));
  Transistor #(.\type ("n"), .gate("br")) transistor_209 (.in(1'b0), .out(W4003), .gate(PHI1));
  Transistor #(.\type ("n"), .gate("br")) transistor_210 (.in(1'b0), .out(W4007), .gate(PHI1));
  Transistor #(.\type ("n"), .gate("br")) transistor_211 (.in(1'b0), .out(W4004), .gate(PHI1));
  Transistor #(.\type ("n"), .gate("br")) transistor_212 (.in(1'b0), .out(W400C), .gate(PHI1));
  Transistor #(.\type ("n"), .gate("br")) transistor_213 (.in(1'b0), .out(W4000), .gate(PHI1));
  Transistor #(.\type ("n"), .gate("br")) transistor_214 (.in(1'b0), .out(W4015), .gate(PHI1));
  Transistor #(.\type ("n"), .gate("br")) transistor_215 (.in(1'b0), .out(W4011), .gate(PHI1));
  Transistor #(.\type ("n"), .gate("br")) transistor_216 (.in(1'b0), .out(W400F), .gate(PHI1));
  Transistor #(.\type ("n"), .gate("br")) transistor_217 (.in(1'b0), .out(W4016), .gate(PHI1));
  Transistor #(.\type ("n"), .gate("br")) transistor_218 (.in(1'b0), .out(W4017), .gate(PHI1));

  // Notes on the sheet:
  //   Block5
  //   Block4
  //   Block3
  //   Block2
  //   Block1
  //   Block5
  //   W4003
  //   W4007
  //   Block4
  //   W4004
  //   W400C
  //   W4000
  //   Block3
  //   W4015
  //   W4011
  //   Block2
  //   W400F
  //   R4017
  //   R4016
  //   Block1
  //   W4016
  //   W4017
endmodule
