// Logisim project registerdecoderrev.circ as structural Verilog: 2 circuits, main circuit main
module main (
  input  PHI1,
  input  R_W,
  input  A15,
  input  A14,
  input  A13,
  input  A12,
  input  A11,
  input  A10,
  input  A9,
  input  A8,
  input  A7,
  input  A6,
  input  A5,
  input  A4,
  input  A3,
  input  A2,
  input  A1,
  input  A0,
  output W4000,
  output W4001,
  output W4002,
  output W4003,
  output W4004,
  output W4005,
  output W4006,
  output W4007,
  output W4008,
  output W400A,
  output W400B,
  output W400C,
  output W400E,
  output W400F,
  output W4010,
  output W4011,
  output W4012,
  output W4013,
  output W4014,
  output W4015,
  output W4016,
  output W4017,
  output nR4015,
  output nR4016,
  output nR4017
);

  Decoder decoder_1 (
    .PHI1(PHI1), .R_W(R_W), .A15(A15), .A14(A14), .A13(A13), .A12(A12), .A11(A11), .A10(A10), .A09(A9),
    .A08(A8), .A07(A7), .A06(A6), .A05(A5), .A4(A4), .A3(A3), .A2(A2), .A1(A1), .A0(A0), .W4000(W4000),
    .W4001(W4001), .W4002(W4002), .W4003(W4003), .W4004(W4004), .W4005(W4005), .W4006(W4006), .W4007(W4007),
    .W4008(W4008), .W400A(W400A), .W400B(W400B), .W400C(W400C), .W400F(W400F), .W4010(W4010), .W4011(W4011),
    .W4012(W4012), .W4013(W4013), .W4014(W4014), .W4015(W4015), .W4016(W4016), .W4017(W4017),
    .nR4015(nR4015), .nR4016(nR4016), .nR4017(nR4017), .W400E(W400E));
endmodule

module Decoder (
  input  PHI1,
  input  R_W,
  input  A15,
  input  A14,
  input  A13,
  input  A12,
  input  A11,
  input  A10,
  input  A09,
  input  A08,
  input  A07,
  input  A06,
  input  A05,
  input  A4,
  input  A3,
  input  A2,
  input  A1,
  input  A0,
  output W4000,
  output W4001,
  output W4002,
  output W4003,
  output W4004,
  output W4005,
  output W4006,
  output W4007,
  output W4008,
  output W400A,
  output W400B,
  output W400C,
  output W400E,
  output W400F,
  output W4010,
  output W4011,
  output W4012,
  output W4013,
  output W4014,
  output W4015,
  output W4016,
  output W4017,
  output nR4015,
  output nR4016,
  output nR4017
);

  wire nor_1_out, nor_2_out, nor_3_out, nor_4_out, nor_5_out, nor_6_out, nor_7_out, nor_8_out, nor_9_out,
       nor_10_out, nor_11_out, nor_12_out, nor_13_out, nor_14_out, nor_15_out, nor_16_out, nor_17_out,
       nor_18_out, nor_19_out, nor_20_out, nor_21_out, nor_22_out, nor_23_out, nor_24_out, nor_25_out,
       nor_26_out, nor_27_out, not_1_out, not_2_out, not_3_out, not_4_out, not_5_out, not_6_out, not_7_out,
       not_8_out, not_9_out, not_10_out, not_11_out, not_12_out, not_13_out, not_14_out, not_15_out,
       not_16_out, not_17_out, not_18_out, not_19_out, not_20_out, not_21_out, not_22_out, not_23_out,
       not_24_out, not_25_out, not_26_out, not_27_out, not_28_out, not_29_out, not_30_out, not_31_out,
       not_32_out, not_33_out, not_34_out, not_35_out, not_36_out, not_37_out, not_38_out, not_39_out,
       not_40_out, not_41_out, not_42_out, not_43_out, not_44_out, not_45_out, not_46_out, not_47_out,
       not_48_out, not_49_out, not_50_out, not_51_out, not_52_out, not_53_out, not_54_out, not_55_out,
       not_56_out, not_57_out, not_58_out, not_59_out, not_60_out, not_61_out, not_62_out, not_63_out,
       not_64_out, not_65_out, not_66_out, not_67_out, not_68_out, not_69_out, not_70_out, not_71_out,
       not_72_out, not_73_out, not_74_out, not_75_out, not_76_out, not_77_out, not_78_out, not_79_out,
       not_80_out, not_81_out, not_82_out, not_83_out;

  not not_1 (not_1_out, A14);
  not not_2 (not_2_out, R_W);
  nor nor_1 (nor_1_out, A15, not_1_out, A13, A12, A11, A10, A09, A08, A07, A06, A05, R_W);
  nor nor_2 (nor_2_out, A15, not_1_out, A13, A12, A11, A10, A09, A08, A07, A06, A05, not_2_out);
  not not_3 (not_3_out, nor_1_out);
  not not_4 (not_4_out, nor_2_out);
  not not_5 (not_5_out, A0);
  not not_6 (not_6_out, A1);
  not not_7 (not_7_out, A0);
  not not_8 (not_8_out, A1);
  not not_9 (not_9_out, A2);
  not not_10 (not_10_out, A0);
  not not_11 (not_11_out, A2);
  not not_12 (not_12_out, A1);
  not not_13 (not_13_out, A2);
  not not_14 (not_14_out, A0);
  not not_15 (not_15_out, A1);
  not not_16 (not_16_out, A2);
  not not_17 (not_17_out, A3);
  not not_18 (not_18_out, A1);
  not not_19 (not_19_out, A3);
  not not_20 (not_20_out, A0);
  not not_21 (not_21_out, A1);
  not not_22 (not_22_out, A3);
  not not_23 (not_23_out, A2);
  not not_24 (not_24_out, A3);
  not not_25 (not_25_out, A1);
  not not_26 (not_26_out, A2);
  not not_27 (not_27_out, A3);
  not not_28 (not_28_out, A0);
  not not_29 (not_29_out, A1);
  not not_30 (not_30_out, A2);
  not not_31 (not_31_out, A3);
  not not_32 (not_32_out, A4);
  not not_33 (not_33_out, A0);
  not not_34 (not_34_out, A4);
  not not_35 (not_35_out, A1);
  not not_36 (not_36_out, A4);
  not not_37 (not_37_out, A0);
  not not_38 (not_38_out, A1);
  not not_39 (not_39_out, A4);
  not not_40 (not_40_out, A2);
  not not_41 (not_41_out, A4);
  not not_42 (not_42_out, A0);
  not not_43 (not_43_out, A2);
  not not_44 (not_44_out, A4);
  not not_45 (not_45_out, A1);
  not not_46 (not_46_out, A2);
  not not_47 (not_47_out, A4);
  not not_48 (not_48_out, A0);
  not not_49 (not_49_out, A1);
  not not_50 (not_50_out, A2);
  not not_51 (not_51_out, A4);
  not not_52 (not_52_out, A0);
  not not_53 (not_53_out, A2);
  not not_54 (not_54_out, A4);
  not not_55 (not_55_out, A1);
  not not_56 (not_56_out, A2);
  not not_57 (not_57_out, A4);
  not not_58 (not_58_out, A0);
  not not_59 (not_59_out, A1);
  not not_60 (not_60_out, A2);
  not not_61 (not_61_out, A4);
  nor nor_3 (nor_3_out, A0, A1, A2, A3, A4, not_3_out);
  not not_62 (not_62_out, nor_3_out);
  nor nor_4 (nor_4_out, not_5_out, A1, A2, A3, A4, not_3_out);
  not not_63 (not_63_out, nor_4_out);
  not not_64 (not_64_out, nor_5_out);
  nor nor_5 (nor_5_out, A0, not_6_out, A2, A3, A4, not_3_out);
  nor nor_6 (nor_6_out, not_7_out, not_8_out, A2, A3, A4, not_3_out);
  not not_65 (not_65_out, nor_6_out);
  nor nor_7 (nor_7_out, A0, A1, not_9_out, A3, A4, not_3_out);
  not not_66 (not_66_out, nor_7_out);
  not not_67 (not_67_out, nor_8_out);
  nor nor_8 (nor_8_out, not_10_out, A1, not_11_out, A3, A4, not_3_out);
  not not_68 (not_68_out, nor_9_out);
  nor nor_9 (nor_9_out, A0, not_12_out, not_13_out, A3, A4, not_3_out);
  not not_69 (not_69_out, nor_10_out);
  nor nor_10 (nor_10_out, not_14_out, not_15_out, not_16_out, A3, A4, not_3_out);
  not not_70 (not_70_out, nor_11_out);
  nor nor_11 (nor_11_out, A0, A1, A2, not_17_out, A4, not_3_out);
  not not_71 (not_71_out, nor_12_out);
  nor nor_12 (nor_12_out, A0, not_18_out, A2, not_19_out, A4, not_3_out);
  nor nor_13 (nor_13_out, not_20_out, not_21_out, A2, not_22_out, A4, not_3_out);
  not not_72 (not_72_out, nor_13_out);
  not not_73 (not_73_out, nor_14_out);
  nor nor_14 (nor_14_out, A0, A1, not_23_out, not_24_out, A4, not_3_out);
  nor nor_15 (nor_15_out, A0, not_25_out, not_26_out, not_27_out, A4, not_3_out);
  not not_74 (not_74_out, nor_15_out);
  nor nor_16 (nor_16_out, not_28_out, not_29_out, not_30_out, not_31_out, A4, not_3_out);
  not not_75 (not_75_out, nor_16_out);
  not not_76 (not_76_out, nor_17_out);
  nor nor_17 (nor_17_out, A0, A1, A2, A3, not_32_out, not_3_out);
  not not_77 (not_77_out, nor_18_out);
  nor nor_18 (nor_18_out, not_33_out, A1, A2, A3, not_34_out, not_3_out);
  not not_78 (not_78_out, nor_19_out);
  nor nor_19 (nor_19_out, A0, not_35_out, A2, A3, not_36_out, not_3_out);
  nor nor_20 (nor_20_out, not_37_out, not_38_out, A2, A3, not_39_out, not_3_out);
  not not_79 (not_79_out, nor_20_out);
  not not_80 (not_80_out, nor_21_out);
  nor nor_21 (nor_21_out, A0, A1, not_40_out, A3, not_41_out, not_3_out);
  not not_81 (not_81_out, nor_22_out);
  nor nor_22 (nor_22_out, not_42_out, A1, not_43_out, A3, not_44_out, not_3_out);
  not not_82 (not_82_out, nor_23_out);
  nor nor_23 (nor_23_out, A0, not_45_out, not_46_out, A3, not_47_out, not_3_out);
  not not_83 (not_83_out, nor_24_out);
  nor nor_24 (nor_24_out, not_48_out, not_49_out, not_50_out, A3, not_51_out, not_3_out);
  not not_84 (nR4015, nor_25_out);
  nor nor_25 (nor_25_out, not_52_out, A1, not_53_out, A3, not_54_out, not_4_out);
  not not_85 (nR4016, nor_26_out);
  nor nor_26 (nor_26_out, A0, not_55_out, not_56_out, A3, not_57_out, not_4_out);
  nor nor_27 (nor_27_out, not_58_out, not_59_out, not_60_out, A3, not_61_out, not_4_out);
  not not_86 (nR4017, nor_27_out);
  nor nor_28 (W4000, not_62_out, PHI1);
  nor nor_29 (W4001, not_63_out, PHI1);
  nor nor_30 (W4002, not_64_out, PHI1);
  nor nor_31 (W4003, not_65_out, PHI1);
  nor nor_32 (W4004, not_66_out, PHI1);
  nor nor_33 (W4005, not_67_out, PHI1);
  nor nor_34 (W4006, not_68_out, PHI1);
  nor nor_35 (W4007, not_69_out, PHI1);
  nor nor_36 (W4008, not_70_out, PHI1);
  nor nor_37 (W400A, not_71_out, PHI1);
  nor nor_38 (W400B, not_72_out, PHI1);
  nor nor_39 (W400C, not_73_out, PHI1);
  nor nor_40 (W400E, not_74_out, PHI1);
  nor nor_41 (W400F, not_75_out, PHI1);
  nor nor_42 (W4010, not_76_out, PHI1);
  nor nor_43 (W4011, not_77_out, PHI1);
  nor nor_44 (W4012, not_78_out, PHI1);
  nor nor_45 (W4013, not_79_out, PHI1);
  nor nor_46 (W4014, not_80_out, PHI1);
  nor nor_47 (W4015, not_81_out, PHI1);
  nor nor_48 (W4016, not_82_out, PHI1);
  nor nor_49 (W4017, not_83_out, PHI1);

  // Notes on the sheet:
  //   /Enable write ports
endmodule
