// Logisim project rwpad.circ as structural Verilog: 1 circuit, main circuit main
module main (
  input  R_W,
  input  nRes,
  output R_W_2
);

  wire pull_resistor_1_node, pull_resistor_2_node, pull_resistor_3_node, pull_resistor_4_node,
       pull_resistor_5_node, transistor_3_out, transistor_8_out;

  Pull_Resistor #(.pull(1)) pull_resistor_1 (.node(pull_resistor_1_node));
  Transistor #(.\type ("n")) transistor_1 (.in(1'b0), .out(pull_resistor_1_node), .gate(R_W));
  Transistor #(.\type ("n")) transistor_2 (.in(1'b0), .out(pull_resistor_1_node), .gate(nRes));
  Pull_Resistor #(.pull(1)) pull_resistor_2 (.node(pull_resistor_2_node));
  Transistor #(.\type ("n")) transistor_3 (
    .in(pull_resistor_2_node), .out(transistor_3_out), .gate(pull_resistor_1_node));
  Transistor #(.\type ("n")) transistor_4 (.in(1'b0), .out(transistor_3_out), .gate(nRes));
  Pull_Resistor #(.pull(1)) pull_resistor_3 (.node(pull_resistor_3_node));
  Transistor #(.\type ("n"), .gate("br")) transistor_5 (
    .in(1'b0), .out(pull_resistor_3_node), .gate(pull_resistor_1_node));
  Transistor #(.\type ("n"), .gate("br")) transistor_6 (.in(1'b0), .out(transistor_3_out), .gate(pull_resistor_3_node));
  Transistor #(.\type ("n"), .gate("br")) transistor_7 (.in(1'b0), .out(pull_resistor_3_node), .gate(nRes));
  Pull_Resistor #(.pull(1)) pull_resistor_4 (.node(pull_resistor_4_node));
  Transistor #(.\type ("n")) transistor_8 (
    .in(pull_resistor_4_node), .out(transistor_8_out), .gate(pull_resistor_3_node));
  Transistor #(.\type ("n")) transistor_9 (.in(1'b0), .out(transistor_8_out), .gate(pull_resistor_1_node));
  Transistor #(.\type ("n"), .gate("br")) transistor_10 (.in(1'b0), .out(transistor_8_out), .gate(nRes));
  Pull_Resistor #(.pull(1)) pull_resistor_5 (.node(pull_resistor_5_node));
  Transistor #(.\type ("n")) transistor_11 (.in(pull_resistor_5_node), .out(R_W_2), .gate(transistor_8_out));
  Transistor #(.\type ("n")) transistor_12 (.in(1'b0), .out(R_W_2), .gate(transistor_3_out));

  // Notes on the sheet:
  //   int R/W= R/W pin, tristate if reset
  //   Same for /INP1,2 and out0-2 and address
  //   int Res= /Res pin
  //   M2 is invertor pad
  //   int IRQ=IRQ pin
  //   int NMI= NMI pin
  //   Phi2=M2+ duty compensate
endmodule
