// Logisim project shiftreg.circ as structural Verilog: 1 circuit, main circuit main
module main (
  input  in_1,
  input  in_2,
  input  in_3,
  input  in_4,
  input  in_5,
  input  in_6,
  input  in_7,
  input  in_8,
  input  step,
  input  load,
  input  res,
  output out,
  output out_13,
  output out_14,
  output out_15,
  output out_16,
  output out_17,
  output out_18,
  output out_19
);

  wire clock_1_out, controlled_buffer_1_out, controlled_buffer_2_out, controlled_buffer_3_out,
       controlled_buffer_4_out, controlled_buffer_5_out, controlled_buffer_6_out, controlled_buffer_7_out,
       controlled_buffer_8_out, d_ff_1_qn, d_ff_2_qn, d_ff_3_qn, d_ff_4_qn, d_ff_5_qn, d_ff_6_qn, d_ff_7_qn,
       d_ff_8_qn, d_ff_10_qn, d_ff_11_qn, d_ff_12_qn, d_ff_13_qn, d_ff_14_qn, d_ff_15_qn, d_ff_16_qn,
       not_1_out;

  Clock clock_1 (.out(clock_1_out));
  not not_1 (not_1_out, clock_1_out);
  D_Flip_Flop #(.trigger("high")) d_ff_1 (
    .clk(clock_1_out), .D(d_ff_10_qn), .Qn(d_ff_1_qn));  // open: Q, preset, en, reset
  assign controlled_buffer_1_out = step ? d_ff_1_qn : 1'bz;  // Controlled_Buffer controlled_buffer_1
  D_Flip_Flop #(.trigger("high")) d_ff_2 (
    .clk(clock_1_out), .D(d_ff_11_qn), .Qn(d_ff_2_qn));  // open: Q, preset, en, reset
  assign controlled_buffer_2_out = step ? d_ff_2_qn : 1'bz;  // Controlled_Buffer controlled_buffer_2
  D_Flip_Flop #(.trigger("high")) d_ff_3 (
    .clk(clock_1_out), .D(d_ff_12_qn), .Qn(d_ff_3_qn));  // open: Q, preset, en, reset
  assign controlled_buffer_3_out = step ? d_ff_3_qn : 1'bz;  // Controlled_Buffer controlled_buffer_3
  D_Flip_Flop #(.trigger("high")) d_ff_4 (
    .clk(clock_1_out), .D(d_ff_13_qn), .Qn(d_ff_4_qn));  // open: Q, preset, en, reset
  assign controlled_buffer_4_out = step ? d_ff_4_qn : 1'bz;  // Controlled_Buffer controlled_buffer_4
  D_Flip_Flop #(.trigger("high")) d_ff_5 (
    .clk(clock_1_out), .D(d_ff_14_qn), .Qn(d_ff_5_qn));  // open: Q, preset, en, reset
  assign controlled_buffer_5_out = step ? d_ff_5_qn : 1'bz;  // Controlled_Buffer controlled_buffer_5
  D_Flip_Flop #(.trigger("high")) d_ff_6 (
    .clk(clock_1_out), .D(d_ff_15_qn), .Qn(d_ff_6_qn));  // open: Q, preset, en, reset
  assign controlled_buffer_6_out = step ? d_ff_6_qn : 1'bz;  // Controlled_Buffer controlled_buffer_6
  D_Flip_Flop #(.trigger("high")) d_ff_7 (
    .clk(clock_1_out), .D(d_ff_16_qn), .Qn(d_ff_7_qn));  // open: Q, preset, en, reset
  assign controlled_buffer_7_out = step ? d_ff_7_qn : 1'bz;  // Controlled_Buffer controlled_buffer_7
  D_Flip_Flop #(.trigger("high")) d_ff_8 (.clk(clock_1_out), .D(1'b0), .Qn(d_ff_8_qn));  // open: Q, preset, en, reset
  assign controlled_buffer_8_out = step ? d_ff_8_qn : 1'bz;  // Controlled_Buffer controlled_buffer_8
  assign controlled_buffer_1_out = load ? in_1 : 1'bz;  // Controlled_Buffer controlled_buffer_9
  assign controlled_buffer_2_out = load ? in_2 : 1'bz;  // Controlled_Buffer controlled_buffer_10
  assign controlled_buffer_3_out = load ? in_3 : 1'bz;  // Controlled_Buffer controlled_buffer_11
  assign controlled_buffer_4_out = load ? in_4 : 1'bz;  // Controlled_Buffer controlled_buffer_12
  assign controlled_buffer_5_out = load ? in_5 : 1'bz;  // Controlled_Buffer controlled_buffer_13
  assign controlled_buffer_6_out = load ? in_6 : 1'bz;  // Controlled_Buffer controlled_buffer_14
  assign controlled_buffer_7_out = load ? in_7 : 1'bz;  // Controlled_Buffer controlled_buffer_15
  assign controlled_buffer_8_out = load ? in_8 : 1'bz;  // Controlled_Buffer controlled_buffer_16
  D_Flip_Flop #(.trigger("high")) d_ff_9 (
    .clk(not_1_out), .D(controlled_buffer_1_out), .Q(out), .reset(res));  // open: Qn, preset, en
  D_Flip_Flop #(.trigger("high")) d_ff_10 (
    .clk(not_1_out), .D(controlled_buffer_2_out), .Q(out_13), .Qn(d_ff_10_qn), .reset(res));  // open: preset, en
  D_Flip_Flop #(.trigger("high")) d_ff_11 (
    .clk(not_1_out), .D(controlled_buffer_3_out), .Q(out_14), .Qn(d_ff_11_qn), .reset(res));  // open: preset, en
  D_Flip_Flop #(.trigger("high")) d_ff_12 (
    .clk(not_1_out), .D(controlled_buffer_4_out), .Q(out_15), .Qn(d_ff_12_qn), .reset(res));  // open: preset, en
  D_Flip_Flop #(.trigger("high")) d_ff_13 (
    .clk(not_1_out), .D(controlled_buffer_5_out), .Q(out_16), .Qn(d_ff_13_qn), .reset(res));  // open: preset, en
  D_Flip_Flop #(.trigger("high")) d_ff_14 (
    .clk(not_1_out), .D(controlled_buffer_6_out), .Q(out_17), .Qn(d_ff_14_qn), .reset(res));  // open: preset, en
  D_Flip_Flop #(.trigger("high")) d_ff_15 (
    .clk(not_1_out), .D(controlled_buffer_7_out), .Q(out_18), .Qn(d_ff_15_qn), .reset(res));  // open: preset, en
  D_Flip_Flop #(.trigger("high")) d_ff_16 (
    .clk(not_1_out), .D(controlled_buffer_8_out), .Q(out_19), .Qn(d_ff_16_qn), .reset(res));  // open: preset, en
endmodule
