// Logisim project spritedmarev.circ as structural Verilog: 6 circuits, main circuit main
module main (
  input  nR4015,
  input  W4014,
  input  D0,
  input  D1,
  input  D2,
  input  D3,
  input  D4,
  input  D5,
  input  D6,
  input  in_10,
  input  D7,
  input  RUNDMC,
  input  in_13,
  input  Z4,
  input  R_W,
  input  RES,
  input  CPUA0,
  input  CPUA1,
  input  CPUA2,
  input  CPUA3,
  input  CPUA4,
  input  CPUA5,
  input  CPUA6,
  input  CPUA7,
  input  CPUA8,
  input  CPUA9,
  input  CPUA10,
  input  CPUA11,
  input  CPUA12,
  input  CPUA13,
  input  CPUA14,
  input  CPUA15,
  input  DMC0,
  input  DMC1,
  input  DMC2,
  input  DMC3,
  input  DMC4,
  input  DMC5,
  input  DMC6,
  input  DMC7,
  input  DMC8,
  input  DMC9,
  input  DMC10,
  input  DMC11,
  input  DMC12,
  input  DMC13,
  input  DMC14,
  output PHI1,
  output PHI2,
  output ACLK,
  output nACLK,
  output R_W__to_R_W_ic_pin,
  output RD,
  output SPRA0,
  output SPRA1,
  output WR,
  output SPRA2,
  output SPRA3,
  output SPRA4,
  output Main_buffer_disable__datapads__disable_1,
  output SPRA5,
  output SPRA6,
  output SPRA7,
  output SPRA8,
  output SPRA9,
  output SPRA10,
  output SPRA11,
  output SPRA12,
  output SPRA13,
  output SPRA14,
  output SPRA15,
  output RDY,
  output CPU_AB,
  output DMC_AB,
  output A0,
  output A1,
  output A2,
  output A3,
  output A4,
  output A5,
  output A6,
  output A7,
  output A8,
  output A9,
  output A10,
  output A11,
  output A12,
  output A13,
  output A14,
  output A15
);

  wire clock_1_out, control_1_spr_cpu, control_1_spr_ppu, control_1_sprs, dmaaddresscounter_1_spre, not_1_out;
  wire [7:0] counter_1_q, ram_1_data, rom_1_data;

  Clock clock_1 (.out(clock_1_out));
  Masterclok masterclok_1 (.PHI0(clock_1_out), .RES(RES), .PHI1(PHI1), .PHI2(PHI2), .ACLK(ACLK), .nACLK(nACLK));
  DMAaddresscounter dmaaddresscounter_1 (
    .ACLK(ACLK), .W4014(W4014), .D0(D0), .D1(D1), .D2(D2), .D3(D3), .D4(D4), .D5(D5), .D6(D6), .D7(D7),
    .RES(RES), .SPRS(control_1_sprs), .SPR_CPU(control_1_spr_cpu), .SPR_PPU(control_1_spr_ppu),
    .SPRA0(SPRA0), .SPRA1(SPRA1), .SPRA2(SPRA2), .SPRA3(SPRA3), .SPRA4(SPRA4), .SPRA5(SPRA5), .SPRA6(SPRA6),
    .SPRA7(SPRA7), .SPRA8(SPRA8), .SPRA9(SPRA9), .SPRA10(SPRA10), .SPRA11(SPRA11), .SPRA12(SPRA12),
    .SPRA13(SPRA13), .SPRA14(SPRA14), .SPRA15(SPRA15), .SPRE(dmaaddresscounter_1_spre), .nACLK(nACLK));
  Control control_1 (
    .PHI1(PHI1), .nACLK(nACLK), .W4014(W4014), .SPRE(dmaaddresscounter_1_spre), .RUNDMC(RUNDMC),
    .in_7(in_13), .R_W(R_W), .RES(RES), .SPRS(control_1_sprs), .RDY(RDY), .SPR_PPU(control_1_spr_ppu),
    .SPR_CPU(control_1_spr_cpu), .ACLK(ACLK));
  AddressMux addressmux_1 (
    .SPR_PPU(control_1_spr_ppu), .SPR_CPU(control_1_spr_cpu), .Z4(Z4), .SPRA0(SPRA0), .CPUA0(CPUA0),
    .DMC0(DMC0), .SPRA1(SPRA1), .CPUA1(CPUA1), .DMC1(DMC1), .SPRA2(SPRA2), .CPUA2(CPUA2), .DMC2(DMC2),
    .SPRA3(SPRA3), .CPUA3(CPUA3), .DMC3(DMC3), .SPRA4(SPRA4), .CPUA4(CPUA4), .DMC4(DMC4), .SPRA5(SPRA5),
    .CPUA5(CPUA5), .DMC5(DMC5), .SPRA6(SPRA6), .CPUA6(CPUA6), .DMC6(DMC6), .SPRA7(SPRA7), .CPUA7(CPUA7),
    .DMC7(DMC7), .SPRA8(SPRA8), .CPUA8(CPUA8), .DMC8(DMC8), .SPRA9(SPRA9), .CPUA9(CPUA9), .DMC9(DMC9),
    .SPRA10(SPRA10), .CPUA10(CPUA10), .DMC10(DMC10), .SPRA11(SPRA11), .CPUA11(CPUA11), .DMC11(DMC11),
    .SPRA12(SPRA12), .CPUA12(CPUA12), .DMC12(DMC12), .SPRA13(SPRA13), .CPUA13(CPUA13), .DMC13(DMC13),
    .SPRA14(SPRA14), .CPUA14(CPUA14), .DMC14(DMC14), .SPRA15(SPRA15), .CPUA15(CPUA15), .CPU_AB(CPU_AB),
    .DMC_AB(DMC_AB), .A0(A0), .A1(A1), .A2(A2), .A3(A3), .A4(A4), .A5(A5), .A6(A6), .A7(A7), .A8(A8),
    .A9(A9), .A10(A10), .A11(A11), .A12(A12), .A13(A13), .A14(A14), .A15(A15));
  Counter #(.trigger("falling")) counter_1 (
    .Q(counter_1_q), .clk(control_1_spr_ppu), .clr(in_10));  // open: load, D, count, carry
  ROM rom_1 (.addr({A7, A6, A5, A4, A3, A2, A1, A0}), .data(rom_1_data), .sel(control_1_spr_cpu));
  RAM #(.bus("asynch")) ram_1 (.addr(counter_1_q), .data(ram_1_data), .sel(control_1_spr_ppu), .ld(1'b0), .clr(in_10));
  DMAbuffer dmabuffer_1 (
    .PHI2(PHI2), .SPR_PPU(control_1_spr_ppu), .D0I(rom_1_data[0]), .D0O(ram_1_data[0]), .D1I(rom_1_data[1]),
    .D1O(ram_1_data[1]), .D2I(rom_1_data[2]), .D2O(ram_1_data[2]), .D3I(rom_1_data[3]), .D3O(ram_1_data[3]),
    .D4I(rom_1_data[4]), .D4O(ram_1_data[4]), .D5I(rom_1_data[5]), .D5O(ram_1_data[5]), .D6I(rom_1_data[6]),
    .D6O(ram_1_data[6]), .D7I(rom_1_data[7]), .D7O(ram_1_data[7]), .R_W(R_W), .nR4015(nR4015),
    ._2R_W(R_W__to_R_W_ic_pin), .WR(WR), .SPR_CPU(control_1_spr_cpu));
  not not_1 (not_1_out, R_W__to_R_W_ic_pin);
  not not_2 (RD, not_1_out);
  and and_1 (Main_buffer_disable__datapads__disable_1, RD, WR);

  // Notes on the sheet:
  //   contents of rom_1 (hex, n*v repeats v):
  //   18 ff 23 58 51 20 0 6d 51 21 0 75 59 22 0 6d 59 23 0 75 61 24 0 6d 61 25 0 75 69 26 0 6d 69 27 0 75
  //   f8 0 0 0 f8 a0 41 d6 f8 fc 41 de f8 fc 43 b7 f8 fc 43 bf f8 71 43 b7 f8 70 43 bf f8 73 43 b7 f8 72
  //   43 bf f8 fc 43 ce f8 fc 43 d6 f8 71 43 ce f8 70 43 d6 f8 73 43 ce f8 72 43 d6 f8 a5 41 d6 f8 fc 41
  //   de f8 a7 41 d6 f8 a6 41 de f8 a9 41 d6 f8 a8 41 de f8 d9 1 15 f8 d9 41 1d f8 0 0 0 f8 0 0 0 b8 fc 43
  //   b6 b8 fc 43 be c0 71 43 b6 c0 70 43 be c8 73 43 b6 c8 72 43 be b8 fc 43 cd b8 fc 43 d5 c0 71 43 cd
  //   c0 70 43 d5 c8 73 43 cd c8 72 43 d5 f8 a5 41 d5 f8 fc 41 dd f8 a7 41 d5 f8 a6 41 dd f8 a9 41 d5 f8
  //   a8 41 dd f8 fc 3 b7 f8 fc 3 bf f8 70 3 b7 f8 71 3 bf f8 72 3 b7 f8 73 3 bf f8 fc 3 ce f8 fc 3 d6 f8
  //   70 3 ce f8 71 3 d6 f8 72 3 ce f8 73 3 d6
  //   If /R4015 (read 4015) then disable data buffer (2a03 databus become Z)
  //   Databus control
endmodule

module DMAaddresscounter (
  input  nACLK,
  input  ACLK,
  input  W4014,
  input  D0,
  input  D1,
  input  D2,
  input  D3,
  input  D4,
  input  D5,
  input  D6,
  input  D7,
  input  RES,
  input  SPRS,
  input  SPR_CPU,
  input  SPR_PPU,
  output SPRA0,
  output SPRA1,
  output SPRA2,
  output SPRA3,
  output SPRA4,
  output SPRA5,
  output SPRA6,
  output SPRA7,
  output SPRA8,
  output SPRA9,
  output SPRA10,
  output SPRA11,
  output SPRA12,
  output SPRA13,
  output SPRA14,
  output SPRA15,
  output SPRE
);

  wire and_1_out, d_ff_1_q, d_ff_1_qn, d_ff_2_q, d_ff_2_qn, d_ff_3_q, d_ff_3_qn, d_ff_4_q, d_ff_4_qn,
       d_ff_5_q, d_ff_5_qn, d_ff_6_q, d_ff_6_qn, d_ff_7_q, d_ff_7_qn, d_ff_8_q, d_ff_8_qn, d_ff_9_q,
       d_ff_10_q, d_ff_11_q, d_ff_12_q, d_ff_13_q, d_ff_14_q, d_ff_15_q, d_ff_16_q, d_ff_17_qn, d_ff_18_qn,
       d_ff_19_qn, d_ff_20_qn, d_ff_21_qn, d_ff_22_qn, d_ff_23_qn, d_ff_24_qn, multiplexer_1_out,
       multiplexer_2_out, multiplexer_3_out, multiplexer_4_out, multiplexer_5_out, multiplexer_6_out,
       multiplexer_7_out, multiplexer_8_out, nor_1_out, nor_2_out, nor_3_out, nor_4_out, nor_5_out,
       nor_6_out, nor_7_out, not_1_out, not_2_out, not_3_out, not_4_out, not_5_out, not_6_out, not_7_out,
       not_8_out, or_1_out, or_2_out, or_3_out, or_4_out, or_5_out, or_6_out, or_7_out, or_8_out;

  or or_1 (or_1_out, W4014, RES);
  or or_2 (or_2_out, W4014, RES);
  or or_3 (or_3_out, W4014, RES);
  or or_4 (or_4_out, W4014, RES);
  or or_5 (or_5_out, W4014, RES);
  or or_6 (or_6_out, W4014, RES);
  or or_7 (or_7_out, W4014, RES);
  or or_8 (or_8_out, W4014, RES);
  and and_1 (and_1_out, ACLK, W4014);
  D_Flip_Flop d_ff_1 (.clk(SPRS), .D(d_ff_17_qn), .Q(d_ff_1_q), .Qn(d_ff_1_qn), .reset(or_1_out));  // open: preset, en
  D_Flip_Flop d_ff_2 (.clk(SPRS), .D(d_ff_18_qn), .Q(d_ff_2_q), .Qn(d_ff_2_qn), .reset(or_2_out));  // open: preset, en
  D_Flip_Flop d_ff_3 (.clk(SPRS), .D(d_ff_19_qn), .Q(d_ff_3_q), .Qn(d_ff_3_qn), .reset(or_3_out));  // open: preset, en
  D_Flip_Flop d_ff_4 (.clk(SPRS), .D(d_ff_20_qn), .Q(d_ff_4_q), .Qn(d_ff_4_qn), .reset(or_4_out));  // open: preset, en
  D_Flip_Flop d_ff_5 (.clk(SPRS), .D(d_ff_21_qn), .Q(d_ff_5_q), .Qn(d_ff_5_qn), .reset(or_5_out));  // open: preset, en
  D_Flip_Flop d_ff_6 (.clk(SPRS), .D(d_ff_22_qn), .Q(d_ff_6_q), .Qn(d_ff_6_qn), .reset(or_6_out));  // open: preset, en
  D_Flip_Flop d_ff_7 (.clk(SPRS), .D(d_ff_23_qn), .Q(d_ff_7_q), .Qn(d_ff_7_qn), .reset(or_7_out));  // open: preset, en
  D_Flip_Flop d_ff_8 (.clk(SPRS), .D(d_ff_24_qn), .Q(d_ff_8_q), .Qn(d_ff_8_qn), .reset(or_8_out));  // open: preset, en
  D_Flip_Flop #(.trigger("high")) d_ff_9 (.clk(and_1_out), .D(D0), .Q(d_ff_9_q));  // open: Qn, preset, en, reset
  D_Flip_Flop #(.trigger("high")) d_ff_10 (.clk(and_1_out), .D(D1), .Q(d_ff_10_q));  // open: Qn, preset, en, reset
  D_Flip_Flop #(.trigger("high")) d_ff_11 (.clk(and_1_out), .D(D2), .Q(d_ff_11_q));  // open: Qn, preset, en, reset
  D_Flip_Flop #(.trigger("high")) d_ff_12 (.clk(and_1_out), .D(D3), .Q(d_ff_12_q));  // open: Qn, preset, en, reset
  D_Flip_Flop #(.trigger("high")) d_ff_13 (.clk(and_1_out), .D(D4), .Q(d_ff_13_q));  // open: Qn, preset, en, reset
  D_Flip_Flop #(.trigger("high")) d_ff_14 (.clk(and_1_out), .D(D5), .Q(d_ff_14_q));  // open: Qn, preset, en, reset
  D_Flip_Flop #(.trigger("high")) d_ff_15 (.clk(and_1_out), .D(D6), .Q(d_ff_15_q));  // open: Qn, preset, en, reset
  D_Flip_Flop #(.trigger("high")) d_ff_16 (.clk(and_1_out), .D(D7), .Q(d_ff_16_q));  // open: Qn, preset, en, reset
  Multiplexer multiplexer_1 (.in0(d_ff_1_qn), .in1(d_ff_1_q), .out(multiplexer_1_out), .sel(1'b1));  // open: en
  Multiplexer multiplexer_2 (.in0(d_ff_2_qn), .in1(d_ff_2_q), .out(multiplexer_2_out), .sel(nor_1_out));  // open: en
  Multiplexer multiplexer_3 (.in0(d_ff_3_qn), .in1(d_ff_3_q), .out(multiplexer_3_out), .sel(nor_2_out));  // open: en
  Multiplexer multiplexer_4 (.in0(d_ff_4_qn), .in1(d_ff_4_q), .out(multiplexer_4_out), .sel(nor_3_out));  // open: en
  Multiplexer multiplexer_5 (.in0(d_ff_5_qn), .in1(d_ff_5_q), .out(multiplexer_5_out), .sel(nor_4_out));  // open: en
  Multiplexer multiplexer_6 (.in0(d_ff_6_qn), .in1(d_ff_6_q), .out(multiplexer_6_out), .sel(nor_5_out));  // open: en
  Multiplexer multiplexer_7 (.in0(d_ff_7_qn), .in1(d_ff_7_q), .out(multiplexer_7_out), .sel(nor_6_out));  // open: en
  Multiplexer multiplexer_8 (.in0(d_ff_8_qn), .in1(d_ff_8_q), .out(multiplexer_8_out), .sel(nor_7_out));  // open: en
  D_Flip_Flop d_ff_17 (.clk(nACLK), .D(multiplexer_1_out), .Qn(d_ff_17_qn));  // open: Q, preset, en, reset
  not not_1 (not_1_out, 1'b1);
  D_Flip_Flop d_ff_18 (.clk(nACLK), .D(multiplexer_2_out), .Qn(d_ff_18_qn));  // open: Q, preset, en, reset
  not not_2 (not_2_out, nor_1_out);
  D_Flip_Flop d_ff_19 (.clk(nACLK), .D(multiplexer_3_out), .Qn(d_ff_19_qn));  // open: Q, preset, en, reset
  not not_3 (not_3_out, nor_2_out);
  D_Flip_Flop d_ff_20 (.clk(nACLK), .D(multiplexer_4_out), .Qn(d_ff_20_qn));  // open: Q, preset, en, reset
  not not_4 (not_4_out, nor_3_out);
  D_Flip_Flop d_ff_21 (.clk(nACLK), .D(multiplexer_5_out), .Qn(d_ff_21_qn));  // open: Q, preset, en, reset
  not not_5 (not_5_out, nor_4_out);
  D_Flip_Flop d_ff_22 (.clk(nACLK), .D(multiplexer_6_out), .Qn(d_ff_22_qn));  // open: Q, preset, en, reset
  not not_6 (not_6_out, nor_5_out);
  D_Flip_Flop d_ff_23 (.clk(nACLK), .D(multiplexer_7_out), .Qn(d_ff_23_qn));  // open: Q, preset, en, reset
  not not_7 (not_7_out, nor_6_out);
  D_Flip_Flop d_ff_24 (.clk(nACLK), .D(multiplexer_8_out), .Qn(d_ff_24_qn));  // open: Q, preset, en, reset
  not not_8 (not_8_out, nor_7_out);
  nor nor_1 (nor_1_out, d_ff_1_qn, not_1_out);
  nor nor_2 (nor_2_out, d_ff_2_qn, not_2_out);
  nor nor_3 (nor_3_out, d_ff_3_qn, not_3_out);
  nor nor_4 (nor_4_out, d_ff_4_qn, not_4_out);
  nor nor_5 (nor_5_out, d_ff_5_qn, not_5_out);
  nor nor_6 (nor_6_out, d_ff_6_qn, not_6_out);
  nor nor_7 (nor_7_out, d_ff_7_qn, not_7_out);
  nor nor_8 (SPRE, d_ff_8_qn, not_8_out);
  Multiplexer multiplexer_9 (.in0(d_ff_1_q), .in1(1'b0), .out(SPRA0), .sel(SPR_PPU));  // open: en
  Multiplexer multiplexer_10 (.in0(d_ff_2_q), .in1(1'b0), .out(SPRA1), .sel(SPR_PPU));  // open: en
  Multiplexer multiplexer_11 (.in0(d_ff_3_q), .in1(1'b1), .out(SPRA2), .sel(SPR_PPU));  // open: en
  Multiplexer multiplexer_12 (.in0(d_ff_4_q), .in1(1'b0), .out(SPRA3), .sel(SPR_PPU));  // open: en
  Multiplexer multiplexer_13 (.in0(d_ff_5_q), .in1(1'b0), .out(SPRA4), .sel(SPR_PPU));  // open: en
  Multiplexer multiplexer_14 (.in0(d_ff_6_q), .in1(1'b0), .out(SPRA5), .sel(SPR_PPU));  // open: en
  Multiplexer multiplexer_15 (.in0(d_ff_7_q), .in1(1'b0), .out(SPRA6), .sel(SPR_PPU));  // open: en
  Multiplexer multiplexer_16 (.in0(d_ff_8_q), .in1(1'b0), .out(SPRA7), .sel(SPR_PPU));  // open: en
  Multiplexer multiplexer_17 (.in0(d_ff_9_q), .in1(1'b0), .out(SPRA8), .sel(SPR_PPU));  // open: en
  Multiplexer multiplexer_18 (.in0(d_ff_10_q), .in1(1'b0), .out(SPRA9), .sel(SPR_PPU));  // open: en
  Multiplexer multiplexer_19 (.in0(d_ff_11_q), .in1(1'b0), .out(SPRA10), .sel(SPR_PPU));  // open: en
  Multiplexer multiplexer_20 (.in0(d_ff_12_q), .in1(1'b0), .out(SPRA11), .sel(SPR_PPU));  // open: en
  Multiplexer multiplexer_21 (.in0(d_ff_13_q), .in1(1'b0), .out(SPRA12), .sel(SPR_PPU));  // open: en
  Multiplexer multiplexer_22 (.in0(d_ff_14_q), .in1(1'b1), .out(SPRA13), .sel(SPR_PPU));  // open: en
  Multiplexer multiplexer_23 (.in0(d_ff_15_q), .in1(1'b0), .out(SPRA14), .sel(SPR_PPU));  // open: en
  Multiplexer multiplexer_24 (.in0(d_ff_16_q), .in1(1'b0), .out(SPRA15), .sel(SPR_PPU));  // open: en
endmodule

module Control (
  input  ACLK,
  input  PHI1,
  input  nACLK,
  input  W4014,
  input  SPRE,
  input  RUNDMC,
  input  in_7,
  input  R_W,
  input  RES,
  output SPRS,
  output RDY,
  output SPR_PPU,
  output SPR_CPU
);

  wire and_1_out, d_ff_1_q, d_ff_2_q, d_ff_3_qn, nand_1_out, nand_2_out, nor_1_out, nor_2_out, nor_4_out,
       nor_5_out, nor_6_out, nor_9_out, nor_10_out, nor_11_out, not_1_out, not_2_out, not_3_out, not_4_out;

  not not_1 (not_1_out, ACLK);
  not not_2 (not_2_out, PHI1);
  D_Flip_Flop d_ff_1 (.clk(nACLK), .D(SPRE), .Q(d_ff_1_q));  // open: Qn, preset, en, reset
  not not_3 (not_3_out, not_1_out);
  D_Flip_Flop d_ff_2 (.clk(not_1_out), .D(nor_5_out), .Q(d_ff_2_q));  // open: Qn, preset, en, reset
  nand nand_1 (nand_1_out, R_W, not_2_out);
  nor nor_1 (nor_1_out, not_1_out, nor_2_out);
  nor nor_2 (nor_2_out, nor_1_out, nACLK);
  and and_1 (and_1_out, d_ff_1_q, SPRS);
  nor nor_3 (SPRS, not_3_out, RUNDMC, d_ff_3_qn);
  not not_4 (not_4_out, d_ff_3_qn);
  nor nor_4 (nor_4_out, not_4_out, RES, nor_5_out);
  nor nor_5 (nor_5_out, W4014, nor_4_out);
  nor nor_6 (nor_6_out, d_ff_2_q, nand_1_out);
  nor nor_7 (SPR_PPU, RUNDMC, d_ff_3_qn, nor_1_out);
  nor nor_8 (SPR_CPU, RUNDMC, d_ff_3_qn, nor_2_out);
  nor nor_9 (nor_9_out, and_1_out, RES, nor_10_out);
  nor nor_10 (nor_10_out, nor_9_out, nor_6_out);
  nor nor_11 (nor_11_out, not_4_out, nor_4_out);
  D_Flip_Flop d_ff_3 (.clk(nACLK), .D(nor_9_out), .Qn(d_ff_3_qn));  // open: Q, preset, en, reset
  nand nand_2 (nand_2_out, nor_11_out, in_7);
  not not_5 (RDY, nand_2_out);

  // Notes on the sheet:
  //   /ACLK2
  //   INV2
  //   DL2
  //   INV4
  //   INV3
  //   DL1
  //   NAND2
  //   NORFF1
  //   RS3
  //   NORFF2
  //   NOR6
  //   NORFF1
  //   RS2
  //   NORFF2
  //   NORFF1
  //   RS1
  //   NORFF2
  //   NOR4
  //   NOR2
  //   NOR3
  //   DL3
  //   NOR5
endmodule

module DMAbuffer (
  input  SPR_CPU,
  input  nR4015,
  input  R_W,
  input  PHI2,
  input  SPR_PPU,
  input  D0I,
  input  D1I,
  input  D2I,
  input  D3I,
  input  D4I,
  input  D5I,
  input  D6I,
  input  D7I,
  output WR,
  output _2R_W,
  output D0O,
  output D1O,
  output D2O,
  output D3O,
  output D4O,
  output D5O,
  output D6O,
  output D7O
);

  wire d_ff_1_qn, d_ff_2_qn, d_ff_3_qn, d_ff_4_qn, d_ff_5_qn, d_ff_6_qn, d_ff_7_qn, d_ff_8_qn, not_1_out;

  not not_1 (not_1_out, R_W);
  D_Flip_Flop d_ff_1 (.clk(PHI2), .D(D0I), .Qn(d_ff_1_qn), .en(SPR_CPU));  // open: Q, preset, reset
  assign D0O = SPR_PPU ? ~d_ff_1_qn : 1'bz;  // Controlled_Inverter controlled_inverter_1
  nor nor_1 (_2R_W, not_1_out, SPR_PPU);
  D_Flip_Flop d_ff_2 (.clk(PHI2), .D(D1I), .Qn(d_ff_2_qn), .en(SPR_CPU));  // open: Q, preset, reset
  assign D1O = SPR_PPU ? ~d_ff_2_qn : 1'bz;  // Controlled_Inverter controlled_inverter_2
  nand nand_1 (WR, nR4015, _2R_W);
  D_Flip_Flop d_ff_3 (.clk(PHI2), .D(D2I), .Qn(d_ff_3_qn), .en(SPR_CPU));  // open: Q, preset, reset
  assign D2O = SPR_PPU ? ~d_ff_3_qn : 1'bz;  // Controlled_Inverter controlled_inverter_3
  D_Flip_Flop d_ff_4 (.clk(PHI2), .D(D3I), .Qn(d_ff_4_qn), .en(SPR_CPU));  // open: Q, preset, reset
  assign D3O = SPR_PPU ? ~d_ff_4_qn : 1'bz;  // Controlled_Inverter controlled_inverter_4
  D_Flip_Flop d_ff_5 (.clk(PHI2), .D(D4I), .Qn(d_ff_5_qn), .en(SPR_CPU));  // open: Q, preset, reset
  assign D4O = SPR_PPU ? ~d_ff_5_qn : 1'bz;  // Controlled_Inverter controlled_inverter_5
  D_Flip_Flop d_ff_6 (.clk(PHI2), .D(D5I), .Qn(d_ff_6_qn), .en(SPR_CPU));  // open: Q, preset, reset
  assign D5O = SPR_PPU ? ~d_ff_6_qn : 1'bz;  // Controlled_Inverter controlled_inverter_6
  D_Flip_Flop d_ff_7 (.clk(PHI2), .D(D6I), .Qn(d_ff_7_qn), .en(SPR_CPU));  // open: Q, preset, reset
  assign D6O = SPR_PPU ? ~d_ff_7_qn : 1'bz;  // Controlled_Inverter controlled_inverter_7
  D_Flip_Flop d_ff_8 (.clk(PHI2), .D(D7I), .Qn(d_ff_8_qn), .en(SPR_CPU));  // open: Q, preset, reset
  assign D7O = SPR_PPU ? ~d_ff_8_qn : 1'bz;  // Controlled_Inverter controlled_inverter_8

  // Notes on the sheet:
  //   INV1
  //   NOR1
endmodule

module Masterclok (
  input  PHI0,
  input  RES,
  output PHI1,
  output PHI2,
  output ACLK,
  output nACLK
);

  wire d_ff_1_qn, d_ff_2_qn, nor_1_out, nor_2_out, not_2_out;

  not not_1 (PHI1, PHI0);
  not not_2 (not_2_out, PHI1);
  D_Flip_Flop d_ff_1 (.clk(PHI1), .D(nor_1_out), .Qn(d_ff_1_qn));  // open: Q, preset, en, reset
  D_Flip_Flop d_ff_2 (.clk(PHI0), .D(d_ff_1_qn), .Qn(d_ff_2_qn));  // open: Q, preset, en, reset
  nor nor_1 (nor_1_out, d_ff_2_qn, RES);
  nor nor_2 (nor_2_out, nor_1_out, not_2_out);
  nor nor_3 (nACLK, not_2_out, PHI0, d_ff_2_qn);
  not not_3 (ACLK, nor_2_out);

  assign PHI2 = PHI0;

  // Notes on the sheet:
  //   INV1
  //   DL1
  //   DL2
  //   NOR1
  //   NOR2
  //   NOR3
endmodule

module AddressMux (
  input  SPR_PPU,
  input  SPR_CPU,
  input  Z4,
  input  SPRA0,
  input  CPUA0,
  input  DMC0,
  input  SPRA1,
  input  CPUA1,
  input  DMC1,
  input  SPRA2,
  input  CPUA2,
  input  DMC2,
  input  SPRA3,
  input  CPUA3,
  input  DMC3,
  input  SPRA4,
  input  CPUA4,
  input  DMC4,
  input  SPRA5,
  input  CPUA5,
  input  DMC5,
  input  SPRA6,
  input  CPUA6,
  input  DMC6,
  input  SPRA7,
  input  CPUA7,
  input  DMC7,
  input  SPRA8,
  input  CPUA8,
  input  DMC8,
  input  SPRA9,
  input  CPUA9,
  input  DMC9,
  input  SPRA10,
  input  CPUA10,
  input  DMC10,
  input  SPRA11,
  input  CPUA11,
  input  DMC11,
  input  SPRA12,
  input  CPUA12,
  input  DMC12,
  input  SPRA13,
  input  CPUA13,
  input  DMC13,
  input  SPRA14,
  input  CPUA14,
  input  DMC14,
  input  SPRA15,
  input  CPUA15,
  output CPU_AB,
  output DMC_AB,
  output A0,
  output A1,
  output A2,
  output A3,
  output A4,
  output A5,
  output A6,
  output A7,
  output A8,
  output A9,
  output A10,
  output A11,
  output A12,
  output A13,
  output A14,
  output A15
);

  not not_1 (DMC_AB, Z4);
  nor nor_1 (CPU_AB, SPR_PPU, SPR_CPU, DMC_AB);
  Multiplexer #(.select(2)) multiplexer_1 (
    .in0(SPRA0), .in1(CPUA0), .in2(DMC0), .out(A0), .sel({DMC_AB, CPU_AB}));  // open: in3, en
  Multiplexer #(.select(2)) multiplexer_2 (
    .in0(SPRA1), .in1(CPUA1), .in2(DMC1), .out(A1), .sel({DMC_AB, CPU_AB}));  // open: in3, en
  Multiplexer #(.select(2)) multiplexer_3 (
    .in0(SPRA2), .in1(CPUA2), .in2(DMC2), .out(A2), .sel({DMC_AB, CPU_AB}));  // open: in3, en
  Multiplexer #(.select(2)) multiplexer_4 (
    .in0(SPRA3), .in1(CPUA3), .in2(DMC3), .out(A3), .sel({DMC_AB, CPU_AB}));  // open: in3, en
  Multiplexer #(.select(2)) multiplexer_5 (
    .in0(SPRA4), .in1(CPUA4), .in2(DMC4), .out(A4), .sel({DMC_AB, CPU_AB}));  // open: in3, en
  Multiplexer #(.select(2)) multiplexer_6 (
    .in0(SPRA5), .in1(CPUA5), .in2(DMC5), .out(A5), .sel({DMC_AB, CPU_AB}));  // open: in3, en
  Multiplexer #(.select(2)) multiplexer_7 (
    .in0(SPRA6), .in1(CPUA6), .in2(DMC6), .out(A6), .sel({DMC_AB, CPU_AB}));  // open: in3, en
  Multiplexer #(.select(2)) multiplexer_8 (
    .in0(SPRA7), .in1(CPUA7), .in2(DMC7), .out(A7), .sel({DMC_AB, CPU_AB}));  // open: in3, en
  Multiplexer #(.select(2)) multiplexer_9 (
    .in0(SPRA8), .in1(CPUA8), .in2(DMC8), .out(A8), .sel({DMC_AB, CPU_AB}));  // open: in3, en
  Multiplexer #(.select(2)) multiplexer_10 (
    .in0(SPRA9), .in1(CPUA9), .in2(DMC9), .out(A9), .sel({DMC_AB, CPU_AB}));  // open: in3, en
  Multiplexer #(.select(2)) multiplexer_11 (
    .in0(SPRA10), .in1(CPUA10), .in2(DMC10), .out(A10), .sel({DMC_AB, CPU_AB}));  // open: in3, en
  Multiplexer #(.select(2)) multiplexer_12 (
    .in0(SPRA11), .in1(CPUA11), .in2(DMC11), .out(A11), .sel({DMC_AB, CPU_AB}));  // open: in3, en
  Multiplexer #(.select(2)) multiplexer_13 (
    .in0(SPRA12), .in1(CPUA12), .in2(DMC12), .out(A12), .sel({DMC_AB, CPU_AB}));  // open: in3, en
  Multiplexer #(.select(2)) multiplexer_14 (
    .in0(SPRA13), .in1(CPUA13), .in2(DMC13), .out(A13), .sel({DMC_AB, CPU_AB}));  // open: in3, en
  Multiplexer #(.select(2)) multiplexer_15 (
    .in0(SPRA14), .in1(CPUA14), .in2(DMC14), .out(A14), .sel({DMC_AB, CPU_AB}));  // open: in3, en
  Multiplexer #(.select(2)) multiplexer_16 (
    .in0(SPRA15), .in1(CPUA15), .in2(1'b1), .out(A15), .sel({DMC_AB, CPU_AB}));  // open: in3, en

  // Notes on the sheet:
  //   INV1
  //   NOR1
endmodule
