// Logisim project triangle.circ as structural Verilog: 5 circuits, main circuit main
module main (
  input  W4008,
  input  W400A,
  input  W400B,
  input  D0,
  input  D1,
  input  D2,
  input  D3,
  input  D4,
  input  D5,
  input  D6,
  input  D7,
  input  RES,
  input  nLFO1,
  input  NOTRI,
  output PHI1,
  output PHI2,
  output ACLK,
  output nACLK,
  output TRI0,
  output TRI1,
  output TRI2,
  output TRI3,
  output TRI_LC
);

  wire clock_1_out, divider_1_fout, linearcounter_1_out, nor_1_out, not_1_out;
  wire [11:0] counter_1_q, register_2_q;
  wire [15:0] counter_2_q, register_1_q;

  Clock clock_1 (.out(clock_1_out));
  Masterclock masterclock_1 (.PHI0(clock_1_out), .RES(RES), .PHI1(PHI1), .PHI2(PHI2), .ACLK(ACLK), .nACLK(nACLK));
  Divider divider_1 (
    .PHI1(PHI1), .PHI2(PHI2), .W400A(W400A), .W400B(W400B), .RES(RES), .D0(D0), .D1(D1), .D2(D2), .D3(D3),
    .D4(D4), .D5(D5), .D6(D6), .D7(D7), .FOUT(divider_1_fout));  // open: FLOAD
  Linearcounter linearcounter_1 (
    .nACLK(nACLK), .ACLK(ACLK), .W4008(W4008), .W400B(W400B), .nLFO1(nLFO1), .RES(RES), .D0(D0), .D1(D1),
    .D2(D2), .D3(D3), .D4(D4), .D5(D5), .D6(D6), .D7(D7), .OUT(linearcounter_1_out), .TRI_LC(TRI_LC));
  Counter #(.width(12), .max('hfff), .trigger("falling")) counter_1 (
    .Q(counter_1_q), .clk(nLFO1), .clr(linearcounter_1_out));  // open: load, D, count, carry
  // Probe on register_1_q
  Counter #(.width(16), .max('hffff)) counter_2 (
    .Q(counter_2_q), .clk(PHI1), .clr(not_1_out));  // open: load, D, count, carry
  Register #(.width(16)) register_1 (.D(counter_2_q), .Q(register_1_q), .clk(not_1_out));  // open: en, clr
  not not_1 (not_1_out, divider_1_fout);
  Register #(.width(12)) register_2 (.D(counter_1_q), .Q(register_2_q), .clk(linearcounter_1_out));  // open: en, clr
  // Probe on register_2_q
  nor nor_1 (nor_1_out, PHI1, linearcounter_1_out, divider_1_fout, NOTRI);
  Output_counter output_counter_1 (
    .PHI1(PHI1), .TSTEP(nor_1_out), .RES(RES), .TRI0(TRI0), .TRI1(TRI1), .TRI2(TRI2), .TRI3(TRI3));

  // Notes on the sheet:
  //   NOR3
endmodule

module Masterclock (
  input  PHI0,
  input  RES,
  output PHI1,
  output PHI2,
  output ACLK,
  output nACLK
);

  wire d_ff_1_qn, d_ff_2_qn, nor_1_out, nor_2_out, not_2_out;

  not not_1 (PHI1, PHI0);
  not not_2 (not_2_out, PHI1);
  D_Flip_Flop d_ff_1 (.clk(PHI1), .D(nor_1_out), .Qn(d_ff_1_qn));  // open: Q, preset, en, reset
  D_Flip_Flop d_ff_2 (.clk(PHI0), .D(d_ff_1_qn), .Qn(d_ff_2_qn));  // open: Q, preset, en, reset
  nor nor_1 (nor_1_out, d_ff_2_qn, RES);
  not not_3 (ACLK, nor_2_out);
  nor nor_2 (nor_2_out, nor_1_out, not_2_out);
  nor nor_3 (nACLK, not_2_out, PHI0, d_ff_2_qn);

  assign PHI2 = PHI0;

  // Notes on the sheet:
  //   INV1
  //   DL1
  //   DL2
  //   NOR1
  //   NOR2
  //   NOR3
endmodule

module Divider (
  input  PHI1,
  input  PHI2,
  input  W400A,
  input  W400B,
  input  RES,
  input  D0,
  input  D1,
  input  D2,
  input  D3,
  input  D4,
  input  D5,
  input  D6,
  input  D7,
  output FLOAD,
  output FOUT
);

  wire and_1_out, and_2_out, and_3_out, and_4_out, and_5_out, and_6_out, and_7_out, and_8_out, and_9_out,
       and_10_out, and_11_out, and_12_out, and_13_out, and_14_out, and_15_out, and_16_out, and_17_out,
       and_18_out, and_19_out, and_20_out, and_21_out, and_22_out, and_23_out, and_24_out, d_ff_1_q,
       d_ff_2_q, d_ff_3_q, d_ff_4_q, d_ff_5_q, d_ff_6_q, d_ff_7_q, d_ff_8_q, d_ff_9_q, d_ff_10_q, d_ff_11_q,
       d_ff_12_q, d_ff_12_qn, d_ff_13_q, d_ff_13_qn, d_ff_14_q, d_ff_14_qn, d_ff_15_q, d_ff_15_qn, d_ff_16_q,
       d_ff_16_qn, d_ff_17_q, d_ff_17_qn, d_ff_18_q, d_ff_18_qn, d_ff_19_q, d_ff_19_qn, d_ff_20_q,
       d_ff_20_qn, d_ff_21_q, d_ff_21_qn, d_ff_22_q, d_ff_22_qn, d_ff_23_qn, d_ff_24_qn, d_ff_25_qn,
       d_ff_26_qn, d_ff_27_qn, d_ff_28_qn, d_ff_29_qn, d_ff_30_qn, d_ff_31_qn, d_ff_32_qn, d_ff_33_qn,
       multiplexer_1_out, multiplexer_2_out, multiplexer_3_out, multiplexer_4_out, multiplexer_5_out,
       multiplexer_6_out, multiplexer_7_out, multiplexer_8_out, multiplexer_9_out, multiplexer_10_out,
       multiplexer_11_out, nor_1_out, nor_3_out, nor_4_out, nor_5_out, nor_6_out, nor_7_out, nor_8_out,
       nor_9_out, nor_10_out, nor_11_out, nor_12_out, nor_13_out, not_1_out, not_2_out, not_3_out, not_4_out,
       not_5_out, not_6_out, not_7_out, not_8_out, not_9_out, not_10_out, not_11_out, not_12_out, not_13_out,
       not_14_out, not_15_out, not_16_out, not_17_out, not_18_out, not_19_out, not_20_out, not_21_out,
       not_22_out, not_23_out, or_1_out, or_2_out, or_3_out, or_4_out, or_5_out, or_6_out, or_7_out,
       or_8_out, or_9_out, or_10_out, or_11_out;

  and and_1 (and_1_out, PHI2, W400A);
  and and_2 (and_2_out, PHI2, W400B);
  D_Flip_Flop #(.trigger("high")) d_ff_1 (.clk(and_1_out), .D(D0), .Q(d_ff_1_q));  // open: Qn, preset, en, reset
  D_Flip_Flop #(.trigger("high")) d_ff_2 (.clk(and_1_out), .D(D1), .Q(d_ff_2_q));  // open: Qn, preset, en, reset
  D_Flip_Flop #(.trigger("high")) d_ff_3 (.clk(and_1_out), .D(D2), .Q(d_ff_3_q));  // open: Qn, preset, en, reset
  D_Flip_Flop #(.trigger("high")) d_ff_4 (.clk(and_1_out), .D(D3), .Q(d_ff_4_q));  // open: Qn, preset, en, reset
  D_Flip_Flop #(.trigger("high")) d_ff_5 (.clk(and_1_out), .D(D4), .Q(d_ff_5_q));  // open: Qn, preset, en, reset
  D_Flip_Flop #(.trigger("high")) d_ff_6 (.clk(and_1_out), .D(D5), .Q(d_ff_6_q));  // open: Qn, preset, en, reset
  D_Flip_Flop #(.trigger("high")) d_ff_7 (.clk(and_1_out), .D(D6), .Q(d_ff_7_q));  // open: Qn, preset, en, reset
  D_Flip_Flop #(.trigger("high")) d_ff_8 (.clk(and_1_out), .D(D7), .Q(d_ff_8_q));  // open: Qn, preset, en, reset
  D_Flip_Flop #(.trigger("high")) d_ff_9 (.clk(and_2_out), .D(D0), .Q(d_ff_9_q));  // open: Qn, preset, en, reset
  D_Flip_Flop #(.trigger("high")) d_ff_10 (.clk(and_2_out), .D(D1), .Q(d_ff_10_q));  // open: Qn, preset, en, reset
  D_Flip_Flop #(.trigger("high")) d_ff_11 (.clk(and_2_out), .D(D2), .Q(d_ff_11_q));  // open: Qn, preset, en, reset
  not not_1 (not_1_out, d_ff_1_q);
  not not_2 (not_2_out, d_ff_2_q);
  not not_3 (not_3_out, d_ff_3_q);
  not not_4 (not_4_out, d_ff_4_q);
  not not_5 (not_5_out, d_ff_5_q);
  not not_6 (not_6_out, d_ff_6_q);
  not not_7 (not_7_out, d_ff_7_q);
  not not_8 (not_8_out, d_ff_8_q);
  not not_9 (not_9_out, d_ff_9_q);
  not not_10 (not_10_out, d_ff_10_q);
  not not_11 (not_11_out, d_ff_11_q);
  and and_3 (and_3_out, FLOAD, d_ff_1_q);
  and and_4 (and_4_out, FLOAD, not_1_out);
  and and_5 (and_5_out, FLOAD, d_ff_2_q);
  and and_6 (and_6_out, FLOAD, not_2_out);
  and and_7 (and_7_out, FLOAD, d_ff_3_q);
  and and_8 (and_8_out, FLOAD, not_3_out);
  and and_9 (and_9_out, FLOAD, d_ff_4_q);
  and and_10 (and_10_out, FLOAD, not_4_out);
  and and_11 (and_11_out, FLOAD, d_ff_5_q);
  and and_12 (and_12_out, FLOAD, not_5_out);
  and and_13 (and_13_out, FLOAD, d_ff_6_q);
  and and_14 (and_14_out, FLOAD, not_6_out);
  and and_15 (and_15_out, FLOAD, d_ff_7_q);
  and and_16 (and_16_out, FLOAD, not_7_out);
  and and_17 (and_17_out, FLOAD, d_ff_8_q);
  and and_18 (and_18_out, FLOAD, not_8_out);
  and and_19 (and_19_out, FLOAD, d_ff_9_q);
  and and_20 (and_20_out, FLOAD, not_9_out);
  and and_21 (and_21_out, FLOAD, d_ff_10_q);
  and and_22 (and_22_out, FLOAD, not_10_out);
  and and_23 (and_23_out, FLOAD, d_ff_11_q);
  and and_24 (and_24_out, FLOAD, not_11_out);
  D_Flip_Flop d_ff_12 (
    .clk(nor_1_out), .D(d_ff_23_qn), .Q(d_ff_12_q), .Qn(d_ff_12_qn), .preset(and_3_out), .reset(or_1_out));  // open: en
  or or_1 (or_1_out, and_4_out, RES);
  D_Flip_Flop d_ff_13 (
    .clk(nor_1_out), .D(d_ff_24_qn), .Q(d_ff_13_q), .Qn(d_ff_13_qn), .preset(and_5_out), .reset(or_2_out));  // open: en
  or or_2 (or_2_out, and_6_out, RES);
  D_Flip_Flop d_ff_14 (
    .clk(nor_1_out), .D(d_ff_25_qn), .Q(d_ff_14_q), .Qn(d_ff_14_qn), .preset(and_7_out), .reset(or_3_out));  // open: en
  or or_3 (or_3_out, and_8_out, RES);
  D_Flip_Flop d_ff_15 (
    .clk(nor_1_out), .D(d_ff_26_qn), .Q(d_ff_15_q), .Qn(d_ff_15_qn), .preset(and_9_out), .reset(or_4_out));  // open: en
  or or_4 (or_4_out, and_10_out, RES);
  D_Flip_Flop d_ff_16 (
    .clk(nor_1_out), .D(d_ff_27_qn), .Q(d_ff_16_q), .Qn(d_ff_16_qn), .preset(and_11_out), .reset(or_5_out));  // open: en
  or or_5 (or_5_out, and_12_out, RES);
  D_Flip_Flop d_ff_17 (
    .clk(nor_1_out), .D(d_ff_28_qn), .Q(d_ff_17_q), .Qn(d_ff_17_qn), .preset(and_13_out), .reset(or_6_out));  // open: en
  or or_6 (or_6_out, and_14_out, RES);
  D_Flip_Flop d_ff_18 (
    .clk(nor_1_out), .D(d_ff_29_qn), .Q(d_ff_18_q), .Qn(d_ff_18_qn), .preset(and_15_out), .reset(or_7_out));  // open: en
  or or_7 (or_7_out, and_16_out, RES);
  D_Flip_Flop d_ff_19 (
    .clk(nor_1_out), .D(d_ff_30_qn), .Q(d_ff_19_q), .Qn(d_ff_19_qn), .preset(and_17_out), .reset(or_8_out));  // open: en
  or or_8 (or_8_out, and_18_out, RES);
  D_Flip_Flop d_ff_20 (
    .clk(nor_1_out), .D(d_ff_31_qn), .Q(d_ff_20_q), .Qn(d_ff_20_qn), .preset(and_19_out), .reset(or_9_out));  // open: en
  or or_9 (or_9_out, and_20_out, RES);
  D_Flip_Flop d_ff_21 (
    .clk(nor_1_out), .D(d_ff_32_qn), .Q(d_ff_21_q), .Qn(d_ff_21_qn), .preset(and_21_out), .reset(or_10_out));  // open: en
  or or_10 (or_10_out, and_22_out, RES);
  D_Flip_Flop d_ff_22 (
    .clk(nor_1_out), .D(d_ff_33_qn), .Q(d_ff_22_q), .Qn(d_ff_22_qn), .preset(and_23_out), .reset(or_11_out));  // open: en
  or or_11 (or_11_out, and_24_out, RES);
  nor nor_1 (nor_1_out, not_23_out, PHI1);
  nor nor_2 (FLOAD, FOUT, PHI1);
  Multiplexer multiplexer_1 (.in0(d_ff_12_qn), .in1(d_ff_12_q), .out(multiplexer_1_out), .sel(1'b1));  // open: en
  Multiplexer multiplexer_2 (.in0(d_ff_13_qn), .in1(d_ff_13_q), .out(multiplexer_2_out), .sel(nor_3_out));  // open: en
  Multiplexer multiplexer_3 (.in0(d_ff_14_qn), .in1(d_ff_14_q), .out(multiplexer_3_out), .sel(nor_4_out));  // open: en
  Multiplexer multiplexer_4 (.in0(d_ff_15_qn), .in1(d_ff_15_q), .out(multiplexer_4_out), .sel(nor_5_out));  // open: en
  Multiplexer multiplexer_5 (.in0(d_ff_16_qn), .in1(d_ff_16_q), .out(multiplexer_5_out), .sel(nor_6_out));  // open: en
  Multiplexer multiplexer_6 (.in0(d_ff_17_qn), .in1(d_ff_17_q), .out(multiplexer_6_out), .sel(nor_7_out));  // open: en
  Multiplexer multiplexer_7 (.in0(d_ff_18_qn), .in1(d_ff_18_q), .out(multiplexer_7_out), .sel(nor_8_out));  // open: en
  Multiplexer multiplexer_8 (.in0(d_ff_19_qn), .in1(d_ff_19_q), .out(multiplexer_8_out), .sel(nor_9_out));  // open: en
  Multiplexer multiplexer_9 (.in0(d_ff_20_qn), .in1(d_ff_20_q), .out(multiplexer_9_out), .sel(nor_10_out));  // open: en
  Multiplexer multiplexer_10 (
    .in0(d_ff_21_qn), .in1(d_ff_21_q), .out(multiplexer_10_out), .sel(nor_11_out));  // open: en
  Multiplexer multiplexer_11 (
    .in0(d_ff_22_qn), .in1(d_ff_22_q), .out(multiplexer_11_out), .sel(nor_12_out));  // open: en
  D_Flip_Flop d_ff_23 (.clk(PHI1), .D(multiplexer_1_out), .Qn(d_ff_23_qn));  // open: Q, preset, en, reset
  not not_12 (not_12_out, 1'b1);
  D_Flip_Flop d_ff_24 (.clk(PHI1), .D(multiplexer_2_out), .Qn(d_ff_24_qn));  // open: Q, preset, en, reset
  not not_13 (not_13_out, nor_3_out);
  D_Flip_Flop d_ff_25 (.clk(PHI1), .D(multiplexer_3_out), .Qn(d_ff_25_qn));  // open: Q, preset, en, reset
  not not_14 (not_14_out, nor_4_out);
  D_Flip_Flop d_ff_26 (.clk(PHI1), .D(multiplexer_4_out), .Qn(d_ff_26_qn));  // open: Q, preset, en, reset
  not not_15 (not_15_out, nor_5_out);
  D_Flip_Flop d_ff_27 (.clk(PHI1), .D(multiplexer_5_out), .Qn(d_ff_27_qn));  // open: Q, preset, en, reset
  not not_16 (not_16_out, nor_6_out);
  D_Flip_Flop d_ff_28 (.clk(PHI1), .D(multiplexer_6_out), .Qn(d_ff_28_qn));  // open: Q, preset, en, reset
  not not_17 (not_17_out, nor_7_out);
  D_Flip_Flop d_ff_29 (.clk(PHI1), .D(multiplexer_7_out), .Qn(d_ff_29_qn));  // open: Q, preset, en, reset
  not not_18 (not_18_out, nor_8_out);
  D_Flip_Flop d_ff_30 (.clk(PHI1), .D(multiplexer_8_out), .Qn(d_ff_30_qn));  // open: Q, preset, en, reset
  not not_19 (not_19_out, nor_9_out);
  D_Flip_Flop d_ff_31 (.clk(PHI1), .D(multiplexer_9_out), .Qn(d_ff_31_qn));  // open: Q, preset, en, reset
  not not_20 (not_20_out, nor_10_out);
  D_Flip_Flop d_ff_32 (.clk(PHI1), .D(multiplexer_10_out), .Qn(d_ff_32_qn));  // open: Q, preset, en, reset
  not not_21 (not_21_out, nor_11_out);
  D_Flip_Flop d_ff_33 (.clk(PHI1), .D(multiplexer_11_out), .Qn(d_ff_33_qn));  // open: Q, preset, en, reset
  not not_22 (not_22_out, nor_12_out);
  nor nor_3 (nor_3_out, d_ff_12_q, not_12_out);
  nor nor_4 (nor_4_out, d_ff_13_q, not_13_out);
  nor nor_5 (nor_5_out, d_ff_14_q, not_14_out);
  nor nor_6 (nor_6_out, d_ff_15_q, not_15_out);
  nor nor_7 (nor_7_out, d_ff_16_q, not_16_out);
  nor nor_8 (nor_8_out, d_ff_17_q, not_17_out);
  nor nor_9 (nor_9_out, d_ff_18_q, not_18_out);
  nor nor_10 (nor_10_out, d_ff_19_q, not_19_out);
  nor nor_11 (nor_11_out, d_ff_20_q, not_20_out);
  nor nor_12 (nor_12_out, d_ff_21_q, not_21_out);
  nor nor_13 (nor_13_out, d_ff_22_q, not_22_out);
  not not_23 (not_23_out, FOUT);
  D_Flip_Flop d_ff_34 (.clk(PHI1), .D(nor_13_out), .Qn(FOUT));  // open: Q, preset, en, reset

  // Notes on the sheet:
  //   FSTEP
  //   FLOAD
  //   NOR1
  //   NOR2
  //   INV1
  //   DL1
endmodule

module Linearcounter (
  input  nACLK,
  input  ACLK,
  input  W4008,
  input  W400B,
  input  nLFO1,
  input  RES,
  input  D0,
  input  D1,
  input  D2,
  input  D3,
  input  D4,
  input  D5,
  input  D6,
  input  D7,
  output OUT,
  output TRI_LC
);

  wire and_1_out, and_2_out, and_3_out, and_4_out, and_5_out, and_6_out, and_7_out, and_8_out, and_9_out,
       and_10_out, and_11_out, and_12_out, and_13_out, and_14_out, and_15_out, d_ff_1_q, d_ff_2_q, d_ff_3_q,
       d_ff_4_q, d_ff_5_q, d_ff_6_q, d_ff_7_q, d_ff_8_q, d_ff_9_q, d_ff_10_q, d_ff_11_qn, d_ff_12_q,
       d_ff_12_qn, d_ff_13_q, d_ff_13_qn, d_ff_14_q, d_ff_14_qn, d_ff_15_q, d_ff_15_qn, d_ff_16_q,
       d_ff_16_qn, d_ff_17_q, d_ff_17_qn, d_ff_18_q, d_ff_18_qn, d_ff_19_qn, d_ff_20_qn, d_ff_21_qn,
       d_ff_22_qn, d_ff_23_qn, d_ff_24_qn, d_ff_25_qn, d_ff_26_q, multiplexer_1_out, multiplexer_2_out,
       multiplexer_3_out, multiplexer_4_out, multiplexer_5_out, multiplexer_6_out, multiplexer_7_out,
       nor_1_out, nor_2_out, nor_3_out, nor_4_out, nor_5_out, nor_6_out, nor_7_out, nor_8_out, nor_9_out,
       nor_10_out, nor_12_out, not_1_out, not_2_out, not_3_out, not_4_out, not_5_out, not_6_out, not_7_out,
       not_8_out, not_9_out, not_10_out, not_11_out, not_12_out, not_13_out, not_14_out, or_1_out, or_2_out,
       or_3_out, or_4_out, or_5_out, or_6_out, or_7_out;

  and and_1 (and_1_out, ACLK, W4008);
  D_Flip_Flop #(.trigger("high")) d_ff_1 (.clk(and_1_out), .D(D0), .Q(d_ff_1_q));  // open: Qn, preset, en, reset
  D_Flip_Flop #(.trigger("high")) d_ff_2 (.clk(and_1_out), .D(D1), .Q(d_ff_2_q));  // open: Qn, preset, en, reset
  D_Flip_Flop #(.trigger("high")) d_ff_3 (.clk(and_1_out), .D(D2), .Q(d_ff_3_q));  // open: Qn, preset, en, reset
  D_Flip_Flop #(.trigger("high")) d_ff_4 (.clk(and_1_out), .D(D3), .Q(d_ff_4_q));  // open: Qn, preset, en, reset
  D_Flip_Flop #(.trigger("high")) d_ff_5 (.clk(and_1_out), .D(D4), .Q(d_ff_5_q));  // open: Qn, preset, en, reset
  D_Flip_Flop #(.trigger("high")) d_ff_6 (.clk(and_1_out), .D(D5), .Q(d_ff_6_q));  // open: Qn, preset, en, reset
  D_Flip_Flop #(.trigger("high")) d_ff_7 (.clk(and_1_out), .D(D6), .Q(d_ff_7_q));  // open: Qn, preset, en, reset
  D_Flip_Flop #(.trigger("high")) d_ff_8 (
    .clk(and_1_out), .D(D7), .Q(d_ff_8_q), .Qn(TRI_LC));  // open: preset, en, reset
  not not_1 (not_1_out, d_ff_1_q);
  not not_2 (not_2_out, d_ff_2_q);
  not not_3 (not_3_out, d_ff_3_q);
  not not_4 (not_4_out, d_ff_4_q);
  not not_5 (not_5_out, d_ff_5_q);
  not not_6 (not_6_out, d_ff_6_q);
  not not_7 (not_7_out, d_ff_7_q);
  and and_2 (and_2_out, nor_4_out, d_ff_1_q);
  and and_3 (and_3_out, nor_4_out, not_1_out);
  and and_4 (and_4_out, nor_4_out, d_ff_2_q);
  and and_5 (and_5_out, nor_4_out, not_2_out);
  and and_6 (and_6_out, nor_4_out, d_ff_3_q);
  and and_7 (and_7_out, nor_4_out, not_3_out);
  and and_8 (and_8_out, nor_4_out, d_ff_4_q);
  and and_9 (and_9_out, nor_4_out, not_4_out);
  and and_10 (and_10_out, nor_4_out, d_ff_5_q);
  and and_11 (and_11_out, nor_4_out, not_5_out);
  and and_12 (and_12_out, nor_4_out, d_ff_6_q);
  and and_13 (and_13_out, nor_4_out, not_6_out);
  and and_14 (and_14_out, nor_4_out, d_ff_7_q);
  and and_15 (and_15_out, nor_4_out, not_7_out);
  D_Flip_Flop d_ff_9 (.clk(nACLK), .D(OUT), .Q(d_ff_9_q));  // open: Qn, preset, en, reset
  D_Flip_Flop d_ff_10 (.clk(nACLK), .D(nor_2_out), .Q(d_ff_10_q));  // open: Qn, preset, en, reset
  D_Flip_Flop d_ff_11 (.clk(nACLK), .D(nor_2_out), .Qn(d_ff_11_qn));  // open: Q, preset, en, reset
  D_Flip_Flop d_ff_12 (
    .clk(nor_3_out), .D(d_ff_19_qn), .Q(d_ff_12_q), .Qn(d_ff_12_qn), .preset(and_2_out), .reset(or_1_out));  // open: en
  or or_1 (or_1_out, and_3_out, RES);
  D_Flip_Flop d_ff_13 (
    .clk(nor_3_out), .D(d_ff_20_qn), .Q(d_ff_13_q), .Qn(d_ff_13_qn), .preset(and_4_out), .reset(or_2_out));  // open: en
  or or_2 (or_2_out, and_5_out, RES);
  D_Flip_Flop d_ff_14 (
    .clk(nor_3_out), .D(d_ff_21_qn), .Q(d_ff_14_q), .Qn(d_ff_14_qn), .preset(and_6_out), .reset(or_3_out));  // open: en
  or or_3 (or_3_out, and_7_out, RES);
  D_Flip_Flop d_ff_15 (
    .clk(nor_3_out), .D(d_ff_22_qn), .Q(d_ff_15_q), .Qn(d_ff_15_qn), .preset(and_8_out), .reset(or_4_out));  // open: en
  or or_4 (or_4_out, and_9_out, RES);
  D_Flip_Flop d_ff_16 (
    .clk(nor_3_out), .D(d_ff_23_qn), .Q(d_ff_16_q), .Qn(d_ff_16_qn), .preset(and_10_out), .reset(or_5_out));  // open: en
  or or_5 (or_5_out, and_11_out, RES);
  D_Flip_Flop d_ff_17 (
    .clk(nor_3_out), .D(d_ff_24_qn), .Q(d_ff_17_q), .Qn(d_ff_17_qn), .preset(and_12_out), .reset(or_6_out));  // open: en
  or or_6 (or_6_out, and_13_out, RES);
  D_Flip_Flop d_ff_18 (
    .clk(nor_3_out), .D(d_ff_25_qn), .Q(d_ff_18_q), .Qn(d_ff_18_qn), .preset(and_14_out), .reset(or_7_out));  // open: en
  or or_7 (or_7_out, and_15_out, RES);
  nor nor_1 (nor_1_out, W400B, nor_2_out);
  nor nor_2 (nor_2_out, nor_1_out, nor_12_out);
  nor nor_3 (nor_3_out, d_ff_9_q, nLFO1, d_ff_10_q);
  nor nor_4 (nor_4_out, nLFO1, d_ff_11_qn);
  Multiplexer multiplexer_1 (.in0(d_ff_12_qn), .in1(d_ff_12_q), .out(multiplexer_1_out), .sel(1'b1));  // open: en
  Multiplexer multiplexer_2 (.in0(d_ff_13_qn), .in1(d_ff_13_q), .out(multiplexer_2_out), .sel(nor_5_out));  // open: en
  Multiplexer multiplexer_3 (.in0(d_ff_14_qn), .in1(d_ff_14_q), .out(multiplexer_3_out), .sel(nor_6_out));  // open: en
  Multiplexer multiplexer_4 (.in0(d_ff_15_qn), .in1(d_ff_15_q), .out(multiplexer_4_out), .sel(nor_7_out));  // open: en
  Multiplexer multiplexer_5 (.in0(d_ff_16_qn), .in1(d_ff_16_q), .out(multiplexer_5_out), .sel(nor_8_out));  // open: en
  Multiplexer multiplexer_6 (.in0(d_ff_17_qn), .in1(d_ff_17_q), .out(multiplexer_6_out), .sel(nor_9_out));  // open: en
  Multiplexer multiplexer_7 (.in0(d_ff_18_qn), .in1(d_ff_18_q), .out(multiplexer_7_out), .sel(nor_10_out));  // open: en
  D_Flip_Flop d_ff_19 (.clk(nACLK), .D(multiplexer_1_out), .Qn(d_ff_19_qn));  // open: Q, preset, en, reset
  not not_8 (not_8_out, 1'b1);
  D_Flip_Flop d_ff_20 (.clk(nACLK), .D(multiplexer_2_out), .Qn(d_ff_20_qn));  // open: Q, preset, en, reset
  not not_9 (not_9_out, nor_5_out);
  D_Flip_Flop d_ff_21 (.clk(nACLK), .D(multiplexer_3_out), .Qn(d_ff_21_qn));  // open: Q, preset, en, reset
  not not_10 (not_10_out, nor_6_out);
  D_Flip_Flop d_ff_22 (.clk(nACLK), .D(multiplexer_4_out), .Qn(d_ff_22_qn));  // open: Q, preset, en, reset
  not not_11 (not_11_out, nor_7_out);
  D_Flip_Flop d_ff_23 (.clk(nACLK), .D(multiplexer_5_out), .Qn(d_ff_23_qn));  // open: Q, preset, en, reset
  not not_12 (not_12_out, nor_8_out);
  D_Flip_Flop d_ff_24 (.clk(nACLK), .D(multiplexer_6_out), .Qn(d_ff_24_qn));  // open: Q, preset, en, reset
  not not_13 (not_13_out, nor_9_out);
  D_Flip_Flop d_ff_25 (.clk(nACLK), .D(multiplexer_7_out), .Qn(d_ff_25_qn));  // open: Q, preset, en, reset
  not not_14 (not_14_out, nor_10_out);
  D_Flip_Flop d_ff_26 (.clk(nACLK), .D(nor_1_out), .Q(d_ff_26_q));  // open: Qn, preset, en, reset
  nor nor_5 (nor_5_out, d_ff_12_q, not_8_out);
  nor nor_6 (nor_6_out, d_ff_13_q, not_9_out);
  nor nor_7 (nor_7_out, d_ff_14_q, not_10_out);
  nor nor_8 (nor_8_out, d_ff_15_q, not_11_out);
  nor nor_9 (nor_9_out, d_ff_16_q, not_12_out);
  nor nor_10 (nor_10_out, d_ff_17_q, not_13_out);
  nor nor_11 (OUT, d_ff_18_q, not_14_out);
  nor nor_12 (nor_12_out, d_ff_26_q, nLFO1, d_ff_8_q);

  // Notes on the sheet:
  //   DL4
  //   DL3
  //   DL2
  //   NORFF1
  //   RS1
  //   NORFF2
  //   NOR5
  //   STEP
  //   NOR4
  //   LOAD
  //   DL5
  //   NOR6
endmodule

module Output_counter (
  input  PHI1,
  input  TSTEP,
  input  RES,
  output TRI0,
  output TRI1,
  output TRI2,
  output TRI3
);

  wire d_ff_1_q, d_ff_1_qn, d_ff_2_q, d_ff_2_qn, d_ff_3_q, d_ff_3_qn, d_ff_4_q, d_ff_4_qn, d_ff_5_q,
       d_ff_5_qn, d_ff_6_qn, d_ff_7_qn, d_ff_8_qn, d_ff_9_qn, d_ff_10_qn, multiplexer_1_out,
       multiplexer_2_out, multiplexer_3_out, multiplexer_4_out, multiplexer_5_out, multiplexer_6_out,
       multiplexer_7_out, multiplexer_8_out, multiplexer_9_out, nor_1_out, nor_2_out, nor_3_out, nor_4_out,
       not_1_out, not_2_out, not_3_out, not_4_out;

  D_Flip_Flop d_ff_1 (.clk(TSTEP), .D(d_ff_6_qn), .Q(d_ff_1_q), .Qn(d_ff_1_qn), .reset(RES));  // open: preset, en
  D_Flip_Flop d_ff_2 (.clk(TSTEP), .D(d_ff_7_qn), .Q(d_ff_2_q), .Qn(d_ff_2_qn), .reset(RES));  // open: preset, en
  D_Flip_Flop d_ff_3 (.clk(TSTEP), .D(d_ff_8_qn), .Q(d_ff_3_q), .Qn(d_ff_3_qn), .reset(RES));  // open: preset, en
  D_Flip_Flop d_ff_4 (.clk(TSTEP), .D(d_ff_9_qn), .Q(d_ff_4_q), .Qn(d_ff_4_qn), .reset(RES));  // open: preset, en
  D_Flip_Flop d_ff_5 (.clk(TSTEP), .D(d_ff_10_qn), .Q(d_ff_5_q), .Qn(d_ff_5_qn), .reset(RES));  // open: preset, en
  Multiplexer multiplexer_1 (.in0(d_ff_1_qn), .in1(d_ff_1_q), .out(multiplexer_1_out), .sel(1'b1));  // open: en
  Multiplexer multiplexer_2 (.in0(d_ff_2_qn), .in1(d_ff_2_q), .out(multiplexer_2_out), .sel(nor_1_out));  // open: en
  Multiplexer multiplexer_3 (.in0(d_ff_3_qn), .in1(d_ff_3_q), .out(multiplexer_3_out), .sel(nor_2_out));  // open: en
  Multiplexer multiplexer_4 (.in0(d_ff_4_qn), .in1(d_ff_4_q), .out(multiplexer_4_out), .sel(nor_3_out));  // open: en
  Multiplexer multiplexer_5 (.in0(d_ff_5_qn), .in1(d_ff_5_q), .out(multiplexer_5_out), .sel(nor_4_out));  // open: en
  D_Flip_Flop d_ff_6 (.clk(PHI1), .D(multiplexer_1_out), .Qn(d_ff_6_qn));  // open: Q, preset, en, reset
  not not_1 (not_1_out, 1'b1);
  D_Flip_Flop d_ff_7 (.clk(PHI1), .D(multiplexer_2_out), .Qn(d_ff_7_qn));  // open: Q, preset, en, reset
  not not_2 (not_2_out, nor_1_out);
  D_Flip_Flop d_ff_8 (.clk(PHI1), .D(multiplexer_3_out), .Qn(d_ff_8_qn));  // open: Q, preset, en, reset
  not not_3 (not_3_out, nor_2_out);
  D_Flip_Flop d_ff_9 (.clk(PHI1), .D(multiplexer_4_out), .Qn(d_ff_9_qn));  // open: Q, preset, en, reset
  not not_4 (not_4_out, nor_3_out);
  D_Flip_Flop d_ff_10 (.clk(PHI1), .D(multiplexer_5_out), .Qn(d_ff_10_qn));  // open: Q, preset, en, reset
  nor nor_1 (nor_1_out, d_ff_1_qn, not_1_out);
  nor nor_2 (nor_2_out, d_ff_2_qn, not_2_out);
  nor nor_3 (nor_3_out, d_ff_3_qn, not_3_out);
  nor nor_4 (nor_4_out, d_ff_4_qn, not_4_out);
  Multiplexer multiplexer_6 (.in0(d_ff_1_q), .in1(d_ff_1_qn), .out(multiplexer_6_out), .sel(d_ff_5_q));  // open: en
  not not_5 (TRI0, multiplexer_6_out);
  Multiplexer multiplexer_7 (.in0(d_ff_2_q), .in1(d_ff_2_qn), .out(multiplexer_7_out), .sel(d_ff_5_q));  // open: en
  not not_6 (TRI1, multiplexer_7_out);
  Multiplexer multiplexer_8 (.in0(d_ff_3_q), .in1(d_ff_3_qn), .out(multiplexer_8_out), .sel(d_ff_5_q));  // open: en
  not not_7 (TRI2, multiplexer_8_out);
  Multiplexer multiplexer_9 (.in0(d_ff_4_q), .in1(d_ff_4_qn), .out(multiplexer_9_out), .sel(d_ff_5_q));  // open: en
  not not_8 (TRI3, multiplexer_9_out);
endmodule
