// Logisim project CounterBit.circ as structural Verilog: 1 circuit, main circuit main
module main (
  input  nACLK,
  input  cin,
  input  LOAD,
  input  RES,
  input  W4003,
  output cout
);

  wire transistor_1_out, transistor_3_out, transistor_6_out, transistor_8_out, transistor_10_out,
       transistor_12_out, transistor_14_out;

  Transistor #(.\type ("n")) transistor_1 (.in(1'b0), .out(transistor_1_out), .gate(RES));
  Transistor #(.\type ("n")) transistor_2 (.in(1'b0), .out(transistor_1_out), .gate(W4003));
  Transistor #(.\type ("n")) transistor_3 (.in(1'b1), .out(transistor_3_out), .gate(1'b1));
  Transistor #(.\type ("n")) transistor_4 (.in(1'b0), .out(transistor_3_out), .gate(transistor_8_out));
  Transistor #(.\type ("n")) transistor_5 (.in(transistor_3_out), .out(transistor_1_out), .gate(LOAD));
  Transistor #(.\type ("n")) transistor_6 (.in(1'b1), .out(transistor_6_out), .gate(1'b1));
  Transistor #(.\type ("n")) transistor_7 (.in(1'b0), .out(transistor_6_out), .gate(transistor_1_out));
  Transistor #(.\type ("n")) transistor_8 (.in(transistor_10_out), .out(transistor_8_out), .gate(nACLK));
  Transistor #(.\type ("n")) transistor_9 (.in(transistor_12_out), .out(transistor_1_out), .gate(nACLK));
  Transistor #(.\type ("n")) transistor_10 (.in(transistor_6_out), .out(transistor_10_out), .gate(transistor_14_out));
  Transistor #(.\type ("n")) transistor_11 (.in(transistor_12_out), .out(transistor_10_out), .gate(cin));
  Transistor #(.\type ("n")) transistor_12 (.in(1'b1), .out(transistor_12_out), .gate(1'b1));
  Transistor #(.\type ("n")) transistor_13 (.in(1'b0), .out(transistor_12_out), .gate(transistor_6_out));
  Transistor #(.\type ("n")) transistor_14 (.in(1'b0), .out(transistor_14_out), .gate(cin));
  Transistor #(.\type ("n")) transistor_15 (.in(1'b0), .out(cout), .gate(transistor_14_out));
  Transistor #(.\type ("n")) transistor_16 (.in(1'b0), .out(cout), .gate(transistor_12_out));
  Transistor #(.\type ("n")) transistor_17 (.in(1'b1), .out(transistor_14_out), .gate(1'b1));
  Transistor #(.\type ("n")) transistor_18 (.in(1'b1), .out(cout), .gate(1'b1));
endmodule
