// Logisim project DMC_DMA_Standalone_Evo.circ as structural Verilog: 26 circuits, main circuit DLatch
module DMC (
  input  ACLK,
  input  n_ACLK,
  input  PHI1,
  input  RES,
  input  RnW,
  input  LOCK,
  input  W4010,
  input  W4011,
  input  W4012,
  input  W4013,
  input  W4015,
  input  n_R4015,
  input  [7:0] Dx_In,
  output n_DMCAB,
  output RUNDMC,
  output DMCRDY,
  output n_DMCINT,
  output [7:0] Dx_Out,
  output [5:0] DMC_Out,
  output [15:0] DMC_Addr
);

  wire dpcm_controlreg_1_irqen, dpcm_controlreg_1_n_loop, dpcm_ctrl_dstep, dpcm_ctrl_nstep, dpcm_ctrl_pcm,
       dpcm_out_dout, sbuf_bout;
  wire [1:0] dpcm_ctrl_bload, dpcm_ctrl_sload;
  wire [2:0] sbcnt_nout;
  wire [3:0] dpcm_controlreg_1_f_out;
  wire [7:0] addr_reg_addr_out, scnt_in_cnt_out;
  wire [8:0] decoder_fr_out;

  DPCM_AddressReg addr_reg (.n_ACLK(n_ACLK), .W4012(W4012), .Dx_In(Dx_In), .Addr_Out(addr_reg_addr_out));
  DPCM_Control dpcm_ctrl (
    .ACLK(ACLK), .n_ACLK(n_ACLK), .PHI1(PHI1), .RES(RES), .RnW(RnW), .LOCK(LOCK), .W4015(W4015),
    .n_R4015(n_R4015), .n_LOOP(dpcm_controlreg_1_n_loop), .IRQEN(dpcm_controlreg_1_irqen),
    .DOUT(dpcm_out_dout), .NOUT(sbcnt_nout[0]), .SOUT(sbcnt_nout[1]), .FLOAD(sbcnt_nout[2]), .Dx_In(Dx_In),
    .n_DMCAB(n_DMCAB), .RUNDMC(RUNDMC), .DMCRDY(DMCRDY), .n_DMCINT(n_DMCINT), .SLOAD(dpcm_ctrl_sload[0]),
    .SSTEP(dpcm_ctrl_sload[1]), .BLOAD(dpcm_ctrl_bload[0]), .BSTEP(dpcm_ctrl_bload[1]),
    .NSTEP(dpcm_ctrl_nstep), .DSTEP(dpcm_ctrl_dstep), .PCM(dpcm_ctrl_pcm), .D4_Out(Dx_Out[4]),
    .D7_Out(Dx_Out[7]));
  DPCM_Output dpcm_out (
    .n_ACLK(n_ACLK), .RES(RES), .W4011(W4011), .BOUT(sbuf_bout), .DSTEP(dpcm_ctrl_dstep), .Dx_In(Dx_In),
    .DMC_Out(DMC_Out), .DOUT(dpcm_out_dout));
  DPCM_Address dpcm_addr (
    .n_ACLK(n_ACLK), .RES(RES), .SLOAD(dpcm_ctrl_sload[0]), .SSTEP(dpcm_ctrl_sload[1]),
    .Addr_In(addr_reg_addr_out), .DMC_Addr(DMC_Addr));
  DPCM_ControlReg dpcm_controlreg_1 (
    .n_ACLK(n_ACLK), .W4010(W4010), .Dx_In(Dx_In), .F_Out(dpcm_controlreg_1_f_out),
    .IRQEN(dpcm_controlreg_1_irqen), .n_LOOP(dpcm_controlreg_1_n_loop));
  DPCM_Decoder decoder (.Fx(dpcm_controlreg_1_f_out), .FR_Out(decoder_fr_out));
  DPCM_SampleCounterIn scnt_in (.n_ACLK(n_ACLK), .W4013(W4013), .Dx_In(Dx_In), .Cnt_Out(scnt_in_cnt_out));
  DPCM_FreqLFSR lfsr (.ACLK(ACLK), .n_ACLK(n_ACLK), .RES(RES), .FR_In(decoder_fr_out), .FLOAD(sbcnt_nout[2]));
  DPCM_SampleCounter scnt (
    .n_ACLK(n_ACLK), .RES(RES), .SLOAD(dpcm_ctrl_sload[0]), .SSTEP(dpcm_ctrl_sload[1]),
    .Cnt_In(scnt_in_cnt_out), .SOUT(sbcnt_nout[1]));
  DPCM_SampleBitCounter sbcnt (.n_ACLK(n_ACLK), .RES(RES), .NSTEP(dpcm_ctrl_nstep), .NOUT(sbcnt_nout[0]));
  DPCM_SampleBuffer sbuf (
    .n_ACLK(n_ACLK), .RES(RES), .BLOAD(dpcm_ctrl_bload[0]), .BSTEP(dpcm_ctrl_bload[1]), .PCM(dpcm_ctrl_pcm),
    .Dx_In(Dx_In), .BOUT(sbuf_bout));
endmodule

module DMA (
  input  ACLK,
  input  n_ACLK,
  input  PHI1,
  input  PHI2,
  input  RES,
  input  RnW,
  input  W4014,
  input  [7:0] Dx_In,
  input  RUNDMC,
  input  n_DMC_AB,
  input  DMCRDY,
  input  [15:0] DMC_Addr,
  input  [15:0] CPU_Addr,
  output [15:0] Ax,
  output [7:0] Dx_Out,
  output RW,
  output RDY
);

  wire addr_lo_endcount, dma_ctrl_spr_cpu, dma_ctrl_spr_ppu, dma_ctrl_sprs, or_1_out;
  wire [7:0] addr_hi_spr_addrhi, addr_lo_spr_addrlo;

  or or_1 (or_1_out, RES, W4014);
  SPRDMA_AddrLowCounter addr_lo (
    .n_ACLK(n_ACLK), .Clear(or_1_out), .Step(dma_ctrl_sprs), .EndCount(addr_lo_endcount),
    .SPR_AddrLo(addr_lo_spr_addrlo));
  SPRDMA_AddrHigh addr_hi (.n_ACLK(n_ACLK), .SetAddr(W4014), .Dx_In(Dx_In), .SPR_AddrHi(addr_hi_spr_addrhi));
  SPRDMA_Control dma_ctrl (
    .ACLK(ACLK), .n_ACLK(n_ACLK), .RES(RES), .W4014(W4014), .RUNDMC(RUNDMC), .SPRE(addr_lo_endcount),
    .PHI1(PHI1), .RnW(RnW), .DMCReady(DMCRDY), .SPRS(dma_ctrl_sprs), .RDY(RDY), .SPR_PPU(dma_ctrl_spr_ppu),
    .SPR_CPU(dma_ctrl_spr_cpu));
  Addr_MUX mux (
    .SPR_CPU(dma_ctrl_spr_cpu), .SPR_PPU(dma_ctrl_spr_ppu), .n_DMC_AB(n_DMC_AB), .DMC_Addr(DMC_Addr),
    .SPR_Addr({addr_hi_spr_addrhi, addr_lo_spr_addrlo}), .CPU_Addr(CPU_Addr), .Ax(Ax));
  SPRDMA_Buffer dma_buf (.SPR_PPU(dma_ctrl_spr_ppu), .PHI2(PHI2), .Dx_In(Dx_In), .RnW(RnW), .Dx_Out(Dx_Out), .RW(RW));
endmodule

module CounterBit (
  input  n_ACLK,
  input  Clear,
  input  Step,
  input  CarryIn,
  output CarryOut,
  output CntOut
);

  wire controlled_buffer_1_out, d_ff_1_qn, latch1_n_valout, multiplexer_1_out, not_1_out;

  assign controlled_buffer_1_out = Clear ? 1'b0 : 1'bz;  // Controlled_Buffer controlled_buffer_1
  assign controlled_buffer_1_out = Step ? latch1_n_valout : 1'bz;  // Controlled_Buffer controlled_buffer_2
  assign controlled_buffer_1_out = n_ACLK ? CntOut : 1'bz;  // Controlled_Buffer controlled_buffer_3
  D_Flip_Flop #(.trigger("high")) d_ff_1 (
    .D(controlled_buffer_1_out), .clk(1'b1), .Q(CntOut), .Qn(d_ff_1_qn));  // open: preset, reset
  Multiplexer multiplexer_1 (.in0(d_ff_1_qn), .in1(CntOut), .out(multiplexer_1_out), .sel(CarryIn));
  DLatch latch1 (.n_ValOut(latch1_n_valout), .Enable(n_ACLK), .Value(multiplexer_1_out));  // open: ValOut
  not not_1 (not_1_out, CarryIn);
  nor nor_1 (CarryOut, not_1_out, d_ff_1_qn);

  // Notes on the sheet:
  //   q
  //   ~q
endmodule

module SPRDMA_AddrLowCounter (
  input  n_ACLK,
  input  Clear,
  input  Step,
  output EndCount,
  output [7:0] SPR_AddrLo
);

  wire counterbit_1_carryout, counterbit_2_carryout, counterbit_3_carryout, counterbit_4_carryout,
       counterbit_5_carryout, counterbit_6_carryout, counterbit_7_carryout;

  CounterBit counterbit_1 (
    .n_ACLK(n_ACLK), .Clear(Clear), .Step(Step), .CarryIn(1'b1), .CarryOut(counterbit_1_carryout),
    .CntOut(SPR_AddrLo[0]));
  CounterBit counterbit_2 (
    .n_ACLK(n_ACLK), .Clear(Clear), .Step(Step), .CarryIn(counterbit_1_carryout),
    .CarryOut(counterbit_2_carryout), .CntOut(SPR_AddrLo[1]));
  CounterBit counterbit_3 (
    .n_ACLK(n_ACLK), .Clear(Clear), .Step(Step), .CarryIn(counterbit_2_carryout),
    .CarryOut(counterbit_3_carryout), .CntOut(SPR_AddrLo[2]));
  CounterBit counterbit_4 (
    .n_ACLK(n_ACLK), .Clear(Clear), .Step(Step), .CarryIn(counterbit_3_carryout),
    .CarryOut(counterbit_4_carryout), .CntOut(SPR_AddrLo[3]));
  CounterBit counterbit_5 (
    .n_ACLK(n_ACLK), .Clear(Clear), .Step(Step), .CarryIn(counterbit_4_carryout),
    .CarryOut(counterbit_5_carryout), .CntOut(SPR_AddrLo[4]));
  CounterBit counterbit_6 (
    .n_ACLK(n_ACLK), .Clear(Clear), .Step(Step), .CarryIn(counterbit_5_carryout),
    .CarryOut(counterbit_6_carryout), .CntOut(SPR_AddrLo[5]));
  CounterBit counterbit_7 (
    .n_ACLK(n_ACLK), .Clear(Clear), .Step(Step), .CarryIn(counterbit_6_carryout),
    .CarryOut(counterbit_7_carryout), .CntOut(SPR_AddrLo[6]));
  CounterBit counterbit_8 (
    .n_ACLK(n_ACLK), .Clear(Clear), .Step(Step), .CarryIn(counterbit_7_carryout), .CarryOut(EndCount),
    .CntOut(SPR_AddrLo[7]));
endmodule

module SPRDMA_AddrHigh (
  input  n_ACLK,
  input  SetAddr,
  input  [7:0] Dx_In,
  output [7:0] SPR_AddrHi
);

  wire [7:0] controlled_buffer_1_out, dlatch_x8_1_n_valout, not_1_out;

  assign controlled_buffer_1_out = n_ACLK ? not_1_out : 8'bz;  // Controlled_Buffer controlled_buffer_1
  assign controlled_buffer_1_out = SetAddr ? Dx_In : 8'bz;  // Controlled_Buffer controlled_buffer_2
  assign not_1_out = ~dlatch_x8_1_n_valout;  // NOT_Gate not_1, 8 bits wide
  DLatch_x8 dlatch_x8_1 (
    .Enable(1'b1), .Value(controlled_buffer_1_out), .ValOut(SPR_AddrHi), .n_ValOut(dlatch_x8_1_n_valout));

  // Notes on the sheet:
  //   x8
  //   FFx8
endmodule

module SPRDMA_Control (
  input  ACLK,
  input  n_ACLK,
  input  RES,
  input  W4014,
  input  RUNDMC,
  input  SPRE,
  input  PHI1,
  input  RnW,
  input  DMCReady,
  output SPRS,
  output RDY,
  output SPR_PPU,
  output SPR_CPU
);

  wire and_1_out, dospr_latch_valout, nand_1_out, nand_2_out, nor_1_out, nor_2_out, nor_4_out, nor_5_out,
       nor_6_out, nor_7_out, nor_10_out, nor_11_out, nospr_latch_n_valout, not_1_out, not_2_out, not_3_out,
       not_4_out, not_5_out, spre_latch_valout;

  not not_1 (not_1_out, ACLK);
  DLatch spre_latch (.ValOut(spre_latch_valout), .Enable(n_ACLK), .Value(SPRE));  // open: n_ValOut
  not not_2 (not_2_out, not_1_out);
  not not_3 (not_3_out, nospr_latch_n_valout);
  nor nor_1 (nor_1_out, not_3_out, RES, nor_2_out);
  nor nor_2 (nor_2_out, W4014, nor_1_out);
  nor nor_3 (SPRS, nospr_latch_n_valout, RUNDMC, not_2_out);
  not not_4 (not_4_out, PHI1);
  nor nor_4 (nor_4_out, not_1_out, nor_5_out);
  nor nor_5 (nor_5_out, n_ACLK, nor_4_out);
  and and_1 (and_1_out, SPRS, spre_latch_valout);
  DLatch dospr_latch (.ValOut(dospr_latch_valout), .Enable(not_1_out), .Value(nor_2_out));  // open: n_ValOut
  nand nand_1 (nand_1_out, not_4_out, RnW);
  not not_5 (not_5_out, nor_5_out);
  DLatch nospr_latch (.n_ValOut(nospr_latch_n_valout), .Enable(n_ACLK), .Value(nor_6_out));  // open: ValOut
  nor nor_6 (nor_6_out, and_1_out, RES, nor_7_out);
  nor nor_7 (nor_7_out, nor_11_out, nor_6_out);
  nor nor_8 (SPR_PPU, nospr_latch_n_valout, RUNDMC, not_5_out);
  nor nor_9 (SPR_CPU, nospr_latch_n_valout, RUNDMC, nor_5_out);
  nor nor_10 (nor_10_out, not_3_out, nor_1_out);
  nor nor_11 (nor_11_out, dospr_latch_valout, nand_1_out);
  nand nand_2 (nand_2_out, nor_10_out, DMCReady);
  not not_6 (RDY, nand_2_out);

  // Notes on the sheet:
  //   SPRE
  //   RUNDMC
  //   RES
  //   W4014
  //   Delayed /ACLK
  //   /ACLK
  //   StartDMA
  //   SPRS
  //   RES
  //   PHI1
  //   R/W
  //   RUNDMC
  //   DMADirToggle
  //   StopDMA
  //   DOSPR
  //   Delayed /ACLK
  //   NOSPR
  //   NOSPR
  //   Increment DMA Addr
  //   DOSPR
  //   DMA Buffer -> PPU
  //   RAM -> DMA Buffer
  //   RDY
  //   DMCRDY
endmodule

module SPRDMA_Buffer (
  input  SPR_PPU,
  input  PHI2,
  input  [7:0] Dx_In,
  input  RnW,
  output [7:0] Dx_Out,
  output RW
);

  wire not_1_out;
  wire [7:0] dlatch_x8_1_n_valout, not_2_out;

  not not_1 (not_1_out, RnW);
  nor nor_1 (RW, SPR_PPU, not_1_out);
  DLatch_x8 dlatch_x8_1 (.Enable(PHI2), .Value(Dx_In), .n_ValOut(dlatch_x8_1_n_valout));  // open: ValOut
  assign not_2_out = ~dlatch_x8_1_n_valout;  // NOT_Gate not_2, 8 bits wide
  assign Dx_Out = SPR_PPU ? not_2_out : 8'bz;  // Controlled_Buffer controlled_buffer_1
endmodule

module Addr_MUX (
  input  SPR_CPU,
  input  SPR_PPU,
  input  n_DMC_AB,
  input  [15:0] DMC_Addr,
  input  [15:0] SPR_Addr,
  input  [15:0] CPU_Addr,
  output [15:0] Ax
);

  wire nor_1_out, not_1_out;
  wire [15:0] controlled_buffer_1_out;

  not not_1 (not_1_out, n_DMC_AB);
  nor nor_1 (nor_1_out, SPR_CPU, SPR_PPU, not_1_out);
  assign controlled_buffer_1_out = not_1_out ? DMC_Addr : 16'bz;  // Controlled_Buffer controlled_buffer_1
  assign controlled_buffer_1_out = SPR_CPU ? SPR_Addr : 16'bz;  // Controlled_Buffer controlled_buffer_2
  assign controlled_buffer_1_out = nor_1_out ? CPU_Addr : 16'bz;  // Controlled_Buffer controlled_buffer_3
  assign controlled_buffer_1_out = SPR_PPU ? 16'h2004 : 16'bz;  // Controlled_Buffer controlled_buffer_4
  assign Ax = controlled_buffer_1_out;  // Buffer buffer_1, 16 bits wide

  // Notes on the sheet:
  //   DMC_AB
  //   CPU_AB (default)
endmodule

module DLatch (
  input  Enable,
  input  Value,
  output ValOut,
  output n_ValOut
);

  D_Flip_Flop #(.trigger("high")) d_ff_1 (.D(Value), .clk(Enable), .Q(ValOut), .Qn(n_ValOut));  // open: preset, reset
endmodule

module DLatch_x8 (
  input  Enable,
  input  [7:0] Value,
  output [7:0] ValOut,
  output [7:0] n_ValOut
);

  Register #(.trigger("high")) register_1 (.D(Value), .en(1'b1), .clk(Enable), .Q(ValOut));  // open: clr
  assign n_ValOut = ~ValOut;  // NOT_Gate not_1, 8 bits wide
endmodule

module DPCM_ControlReg (
  input  n_ACLK,
  input  W4010,
  input  [7:0] Dx_In,
  output [3:0] F_Out,
  output IRQEN,
  output n_LOOP
);
endmodule

module DPCM_IntControl (
  input  RES,
  input  W4015,
  input  n_R4015,
  input  n_LOOP,
  input  ED1,
  output D7_Out,
  output n_DMCINT
);
endmodule

module DPCM_EnableControl (
  input  n_ACLK,
  input  RES,
  input  W4015,
  input  n_R4015,
  input  ED2,
  input  IRQEN,
  input  DMC1,
  input  SOUT,
  input  D4_In,
  output D4_Out,
  output ED1,
  output DMC2
);
endmodule

module DPCM_DMAControl (
  input  ACLK,
  input  n_ACLK,
  input  PHI1,
  input  RnW,
  input  RES,
  input  CTRL1,
  input  CTRL2,
  output DMCRDY,
  output RUNDMC,
  output n_DMCAB
);
endmodule

module DPCM_SampleCounterControl (
  input  ACLK,
  input  n_ACLK,
  input  DMC1,
  input  DMC2,
  input  ED2,
  input  FLOAD,
  output SLOAD,
  output SSTEP,
  output NSTEP,
  output CTRL2
);
endmodule

module DPCM_SampleBufferControl (
  input  ACLK,
  input  n_ACLK,
  input  PHI1,
  input  RES,
  input  LOCK,
  input  FLOAD,
  input  DOUT,
  input  NOUT,
  input  n_DMCAB,
  output BLOAD,
  output BSTEP,
  output PCM,
  output DSTEP,
  output DMC1,
  output CTRL1
);
endmodule

module DPCM_Control (
  input  ACLK,
  input  n_ACLK,
  input  PHI1,
  input  RES,
  input  RnW,
  input  LOCK,
  input  W4015,
  input  n_R4015,
  input  n_LOOP,
  input  IRQEN,
  input  DOUT,
  input  NOUT,
  input  SOUT,
  input  FLOAD,
  input  [7:0] Dx_In,
  output n_DMCAB,
  output RUNDMC,
  output DMCRDY,
  output n_DMCINT,
  output SLOAD,
  output SSTEP,
  output BLOAD,
  output BSTEP,
  output NSTEP,
  output DSTEP,
  output PCM,
  output D4_Out,
  output D7_Out
);

  DPCM_IntControl int_ctrl ();  // open: RES, W4015, n_R4015, n_LOOP, ED1, D7_Out, n_DMCINT
  DPCM_EnableControl enable_ctrl ();  // open: n_ACLK, RES, W4015, n_R4015, ED2, IRQEN, DMC1, SOUT, D4_In, D4_Out, ED1, DMC2
  DPCM_DMAControl dma_ctrl ();  // open: ACLK, n_ACLK, PHI1, RnW, RES, CTRL1, CTRL2, DMCRDY, RUNDMC, n_DMCAB
  DPCM_SampleCounterControl scnt_ctrl ();  // open: ACLK, n_ACLK, DMC1, DMC2, ED2, FLOAD, SLOAD, SSTEP, NSTEP, CTRL2
  DPCM_SampleBufferControl sbuf_ctrl ();  // open: ACLK, n_ACLK, PHI1, RES, LOCK, FLOAD, DOUT, NOUT, n_DMCAB, BLOAD, BSTEP, PCM, DSTEP, DMC1, CTRL1
endmodule

module DPCM_SampleCounterIn (
  input  n_ACLK,
  input  W4013,
  input  [7:0] Dx_In,
  output [7:0] Cnt_Out
);
endmodule

module DPCM_SampleCounter (
  input  n_ACLK,
  input  RES,
  input  SLOAD,
  input  SSTEP,
  input  [7:0] Cnt_In,
  output SOUT
);
endmodule

module DPCM_SampleBuffer (
  input  n_ACLK,
  input  RES,
  input  BLOAD,
  input  BSTEP,
  input  PCM,
  input  [7:0] Dx_In,
  output BOUT
);
endmodule

module DPCM_SampleBitCounter (
  input  n_ACLK,
  input  RES,
  input  NSTEP,
  output NOUT
);
endmodule

module DPCM_Decoder (
  input  [3:0] Fx,
  output [8:0] FR_Out
);
endmodule

module DPCM_FreqLFSR (
  input  ACLK,
  input  n_ACLK,
  input  RES,
  input  [8:0] FR_In,
  output FLOAD
);
endmodule

module DPCM_AddressReg (
  input  n_ACLK,
  input  W4012,
  input  [7:0] Dx_In,
  output [7:0] Addr_Out
);
endmodule

module DPCM_Address (
  input  n_ACLK,
  input  RES,
  input  SLOAD,
  input  SSTEP,
  input  [7:0] Addr_In,
  output [15:0] DMC_Addr
);
endmodule

module DPCM_Output (
  input  n_ACLK,
  input  RES,
  input  W4011,
  input  BOUT,
  input  DSTEP,
  input  [7:0] Dx_In,
  output [5:0] DMC_Out,
  output DOUT
);
endmodule
