// Logisim project NMOS_CheatSheet.circ as structural Verilog
module PlexedTranspLatch (
  input  sel_A,
  input  A,
  input  sel_B,
  input  B,
  input  sel_C,
  input  C,
  output n_val_out,
  output value_out,
  output n_value_out
);

  wire multiplexer_1_out, multiplexer_2_out, multiplexer_3_out, transistor_1_out, undriven;

  Transistor #(.\type ("n")) transistor_1 (.in(A), .out(transistor_1_out), .gate(sel_A));
  Transistor #(.\type ("n")) transistor_2 (.in(B), .out(transistor_1_out), .gate(sel_B));
  // NoConnect on undriven
  Multiplexer multiplexer_1 (.in0(undriven), .in1(A), .out(multiplexer_1_out), .sel(sel_A));
  Transistor #(.\type ("n")) transistor_3 (.in(C), .out(transistor_1_out), .gate(sel_C));
  Multiplexer multiplexer_2 (.in0(multiplexer_1_out), .in1(B), .out(multiplexer_2_out), .sel(sel_B));
  Multiplexer multiplexer_3 (.in0(multiplexer_2_out), .in1(C), .out(multiplexer_3_out), .sel(sel_C));
  Transistor #(.\type ("n")) transistor_4 (.in(1'b0), .out(n_val_out), .gate(transistor_1_out));
  D_Flip_Flop #(.trigger("high")) d_ff_1 (
    .D(multiplexer_3_out), .clk(1'b1), .Q(value_out), .Qn(n_value_out));  // open: preset, reset

  // Notes on the sheet:
  //   Transparent Latch
  //   Transparent Latch
endmodule
