// Logisim project NSFPlayer.circ as structural Verilog: 7 circuits, main circuit NSFPlayer
module NSFPlayer (
  input  nRES,
  input  nIRQ
);

  wire apu_p2, apu_p3, apu_p6, apu_p8, apu_p12, apu_p13, apu_p14, apu_p15, apu_p17, apu_p20, XTAL_out;
  wire [7:0] apu_p9, apu_p10, apu_p18, apu_p19, apu_p21;
  wire [14:0] apu_p22;
  wire [15:0] apu_p7, apu_p16;
  wire [23:0] dumper_addr;
  wire [31:0] dumper_data;

  Clock XTAL (.out(XTAL_out));
  // _2A03_APU apu: pin names not known; wires that end beside it: XTAL_out, apu_p2, apu_p3, nRES, nIRQ, apu_p6, apu_p7, apu_p8, apu_p9, apu_p10, 1'b0, apu_p12, apu_p13, apu_p14, apu_p15, apu_p16, apu_p17, apu_p18, apu_p19, apu_p20, apu_p21, apu_p22
  Pull_Resistor pull_resistor_1 (.node(apu_p12));
  BankedSRAM bank_switcher (
    .M2(apu_p12), .Addr(apu_p16), .Data_in(apu_p19), .R_W(apu_p17), .Data_out(apu_p10), .nNMI(apu_p6),
    .nRES(nRES));
  // MOS_6502 core: pin names not known; wires that end beside it: apu_p13, apu_p20, 1'b1, apu_p14, apu_p15, nRES, apu_p18[0], apu_p18[1], apu_p18[2], apu_p18[3], apu_p18[4], apu_p18[5], apu_p18[6], apu_p18[7], apu_p2, apu_p3, apu_p8, apu_p7[0], apu_p7[1], apu_p7[2], apu_p7[3], apu_p7[4], apu_p7[5], apu_p7[6], apu_p7[7], apu_p7[8], apu_p7[9], apu_p7[10], apu_p7[11], apu_p7[12], apu_p7[13], apu_p7[14], apu_p7[15], apu_p9[0], apu_p9[1], apu_p9[2], apu_p9[3], apu_p9[4], apu_p9[5], apu_p9[6], apu_p9[7]
  AUXDumper dumper (.PHI1(apu_p2), .AUX({1'b0, apu_p22, apu_p21}), .Addr(dumper_addr), .Data(dumper_data));
  RAM #(.addrWidth(24), .dataWidth(32), .bus("asynch")) ram_1 (
    .addr(dumper_addr), .data(dumper_data), .sel(1'b1), .ld(1'b0), .clr(1'b0));

  // Notes on the sheet:
  //   N.C.
  //   <-- Load .nsf here
  //   Taram-param-pam. Pam! Peep, peep, peep. Pipipipip, pip, pibibip
endmodule

module AUXDumper (
  input  PHI1,
  input  [23:0] AUX,
  output [23:0] Addr,
  output [31:0] Data
);

  wire adder_1_p3, counter_2_q, counter_3_q;
  wire [31:0] aux_a_1_a, aux_b_1_a;

  AUX_A aux_a_1 (.d(AUX[7:0]), .a(aux_a_1_a));
  AUX_B aux_b_1 (.d(AUX[23:8]), .a(aux_b_1_a));
  Counter #(.width(23), .max('h7fffff)) counter_1 (.Q(Addr[23:1]), .clk(PHI1));  // open: load, D, count, carry, clr
  Counter #(.width(1), .max('h1)) counter_2 (.Q(counter_2_q), .clk(PHI1));  // open: load, D, count, carry, clr
  Counter #(.width(1), .max('h1), .trigger("falling")) counter_3 (
    .Q(counter_3_q), .clk(PHI1));  // open: load, D, count, carry, clr
  // Adder adder_1: pin names not known; wires that end beside it: aux_a_1_a, aux_b_1_a, adder_1_p3
  // Divider divider_1: pin names not known; wires that end beside it: adder_1_p3, 32'h40000000, Data
  xnor xnor_1 (Addr[0], counter_2_q, counter_3_q);

  // Notes on the sheet:
  //   a + b
  //   The invention of the org to make the ADDR tick EVERY half cycle.
  //    : 2
  //   normalized samples in range [0.0f; 1.0f]
endmodule

module BankedSRAM (
  input  M2,
  input  [15:0] Addr,
  input  [7:0] Data_in,
  input  R_W,
  input  nRES,
  output [7:0] Data_out,
  output nNMI
);

  wire addrdecoder_1_cs_rom, addrdecoder_1_cs_wram, not_1_out, not_2_out;
  wire [15:0] and_1_out;
  wire [23:0] adder_1_out;

  AddrDecoder addrdecoder_1 (
    .Addr(Addr), .CS_WRAM(addrdecoder_1_cs_wram), .CS_ROM(addrdecoder_1_cs_rom));  // open: CS_BSW_REG
  assign and_1_out = Addr & 16'h7fff;  // AND_Gate and_1, 16 bits wide
  Adder #(.width(24)) adder_1 (.a({{8{1'b0}}, and_1_out}), .b(24'h80), .out(adder_1_out), .cin(1'b0));  // open: cout
  not not_1 (not_1_out, R_W);
  not not_2 (not_2_out, nRES);
  NMI_Generator nmi_generator_1 (.M2(M2), .nRES(nRES), .nNMI(nNMI));
  RAM #(.addrWidth(11), .bus("separate")) ram_1 (
    .addr(Addr[10:0]), .din(Data_in), .data(Data_out), .str(not_1_out), .sel(addrdecoder_1_cs_wram),
    .clk(M2), .ld(R_W), .clr(not_2_out));
  RAM #(.addrWidth(24), .bus("asynch")) ram_2 (
    .addr(adder_1_out), .data(Data_out), .sel(addrdecoder_1_cs_rom), .ld(addrdecoder_1_cs_rom));  // open: clr

  // Notes on the sheet:
  //   TBD: Bank switch logic here
  //   WRAM (0x800 bytes)
  //   .nsf file image converted to .hex
  //   <-- Load .nsf here
endmodule

module AUX_A (
  input  [7:0] d,
  output [31:0] a
);

  ROM #(.dataWidth(32)) rom_1 (.addr(d), .data(a), .sel(1'b1));

  // Notes on the sheet:
  //   0...255
endmodule

module AUX_B (
  input  [15:0] d,
  output [31:0] a
);

  ROM #(.addrWidth(15), .dataWidth(32)) rom_1 (.addr(d[14:0]), .data(a), .sel(1'b1));

  // Notes on the sheet:
  //   0...32767
endmodule

module NMI_Generator (
  input  M2,
  input  nRES,
  output nNMI
);


  assign nNMI = 1'b0;
endmodule

module AddrDecoder (
  input  [15:0] Addr,
  output CS_WRAM,
  output CS_ROM,
  output CS_BSW_REG
);

  wire [15:0] and_1_out;

  assign and_1_out = Addr & 16'hfff8;  // AND_Gate and_1, 16 bits wide
  Comparator #(.width(16), .mode("unsigned")) comparator_1 (.a(Addr), .b(16'h800), .lt(CS_WRAM));  // open: gt, eq
  Comparator #(.width(16), .mode("unsigned")) comparator_2 (.a(Addr), .b(16'h7fff), .gt(CS_ROM));  // open: eq, lt
  Comparator #(.width(16), .mode("unsigned")) comparator_3 (
    .a(and_1_out), .b(16'h5ff8), .eq(CS_BSW_REG));  // open: gt, lt
endmodule
