// Logisim project PPUPlayer.circ as structural Verilog: 8 circuits, main circuit PPUPlayer_NTSC
module PPUPlayer_NTSC (
  input  R_W,
  input  [7:0] DB,
  input  [2:0] RS,
  input  nDBE,
  input  nRES
);

  wire CLK_out, n2c02_ntsc_1_ale, n2c02_ntsc_1_nrd, n2c02_ntsc_1_nwr, not_1_out, not_2_out,
       nrom_cartridge_1_nvram_cs, pull_resistor_1_node;
  wire [5:0] n2c02_ntsc_1_pa8;
  wire [7:0] ls373_1_val_out, n2c02_ntsc_1_pa0, n2c02_ntsc_1_pd0_w, nrom_cartridge_1_ppudata_out;
  wire [10:0] n2c02_ntsc_1_vout;
  wire [10:10] nrom_cartridge_1_vram_a10;
  wire [23:0] videodumper_1_addr;
  wire [31:0] videodumper_1_data;

  Clock CLK (.out(CLK_out));
  Pull_Resistor #(.pull(1)) pull_resistor_1 (.node(pull_resistor_1_node));
  _2C02_NTSC u_2c02_ntsc_1 (
    .VOUT(n2c02_ntsc_1_vout), .nRES(nRES), .nINT(pull_resistor_1_node), .nDBE(nDBE), .RS2(RS[2]),
    .RS1(RS[1]), .RS0(RS[0]), .R_W(R_W), .D7(DB[7]), .D6(DB[6]), .D5(DB[5]), .D4(DB[4]), .D3(DB[3]),
    .D2(DB[2]), .D1(DB[1]), .D0(DB[0]), .nRD(n2c02_ntsc_1_nrd), .nWR(n2c02_ntsc_1_nwr),
    .PA13(n2c02_ntsc_1_pa8[5]), .PA12(n2c02_ntsc_1_pa8[4]), .PA11(n2c02_ntsc_1_pa8[3]),
    .PA10(n2c02_ntsc_1_pa8[2]), .PA9(n2c02_ntsc_1_pa8[1]), .PA8(n2c02_ntsc_1_pa8[0]),
    .PA7(n2c02_ntsc_1_pa0[7]), .PA6(n2c02_ntsc_1_pa0[6]), .PA5(n2c02_ntsc_1_pa0[5]),
    .PA4(n2c02_ntsc_1_pa0[4]), .PA3(n2c02_ntsc_1_pa0[3]), .PA2(n2c02_ntsc_1_pa0[2]),
    .PA1(n2c02_ntsc_1_pa0[1]), .PA0(n2c02_ntsc_1_pa0[0]), .ALE(n2c02_ntsc_1_ale),
    .PD7(nrom_cartridge_1_ppudata_out[7]), .PD6(nrom_cartridge_1_ppudata_out[6]),
    .PD5(nrom_cartridge_1_ppudata_out[5]), .PD4(nrom_cartridge_1_ppudata_out[4]),
    .PD3(nrom_cartridge_1_ppudata_out[3]), .PD2(nrom_cartridge_1_ppudata_out[2]),
    .PD1(nrom_cartridge_1_ppudata_out[1]), .PD0(nrom_cartridge_1_ppudata_out[0]),
    .PD7_W(n2c02_ntsc_1_pd0_w[7]), .PD6_W(n2c02_ntsc_1_pd0_w[6]), .PD5_W(n2c02_ntsc_1_pd0_w[5]),
    .PD4_W(n2c02_ntsc_1_pd0_w[4]), .PD3_W(n2c02_ntsc_1_pd0_w[3]), .PD2_W(n2c02_ntsc_1_pd0_w[2]),
    .PD1_W(n2c02_ntsc_1_pd0_w[1]), .PD0_W(n2c02_ntsc_1_pd0_w[0]), .EXT0(1'b0), .EXT1(1'b0), .EXT2(1'b0),
    .EXT3(1'b0), .CLK(CLK_out));  // open: D7_2, D6_2, D5_2, D4_2, D3_2, D2_2, D1_2, D0_2, EXT0_2, EXT1_2, EXT2_2, EXT3_2
  not not_1 (not_1_out, pull_resistor_1_node);
  LED led_1 (.in(not_1_out));
  VideoDumper videodumper_1 (
    .CLK(CLK_out), .VIDEO_IN(n2c02_ntsc_1_vout), .ADDR(videodumper_1_addr), .DATA(videodumper_1_data));
  LS373 ls373_1 (.LE(n2c02_ntsc_1_ale), .nOE(1'b0), .val_in(n2c02_ntsc_1_pa0), .val_out(ls373_1_val_out));
  RAM #(.addrWidth(24), .dataWidth(32), .bus("asynch")) ram_1 (
    .addr(videodumper_1_addr), .data(videodumper_1_data), .sel(1'b1), .ld(1'b0), .clr(1'b0));
  NROM_Cartridge nrom_cartridge_1 (
    .PPUData_In(n2c02_ntsc_1_pd0_w), .nRD(n2c02_ntsc_1_nrd), .nWR(n2c02_ntsc_1_nwr),
    .PPUAddr({n2c02_ntsc_1_pa8, ls373_1_val_out}), .nPA13(not_2_out),
    .PPUData_Out(nrom_cartridge_1_ppudata_out), .nVRAM_CS(nrom_cartridge_1_nvram_cs),
    .VRAM_A10(nrom_cartridge_1_vram_a10[10]), .V_Mirroring(1'b1));
  not not_2 (not_2_out, n2c02_ntsc_1_pa8[5]);
  SRAM sram_1 (
    .nCS(nrom_cartridge_1_nvram_cs), .nWE(n2c02_ntsc_1_nwr), .nOE(n2c02_ntsc_1_nrd),
    .Addr({nrom_cartridge_1_vram_a10[10], n2c02_ntsc_1_pa8[1:0], ls373_1_val_out}),
    .Data_In(n2c02_ntsc_1_pd0_w), .Data_Out(nrom_cartridge_1_ppudata_out));

  // Notes on the sheet:
  //   PA0-7
  //   PPU Data Out
  //   PPU Data In
endmodule

module PPUPlayer_RGB_PPU (
  input  R_W,
  input  [7:0] DB,
  input  [2:0] RS,
  input  nDBE,
  input  nRES
);

  wire CLK_out, n2c04_0003_rgb_1_ale, n2c04_0003_rgb_1_nrd, n2c04_0003_rgb_1_nwr, n2c04_0003_rgb_1_sync,
       not_1_out, not_2_out, nrom_cartridge_1_nvram_cs, pull_resistor_1_node;
  wire [5:0] n2c04_0003_rgb_1_pa8;
  wire [7:0] ls373_1_val_out, n2c04_0003_rgb_1_blue, n2c04_0003_rgb_1_green, n2c04_0003_rgb_1_pa0,
       n2c04_0003_rgb_1_pd0_w, n2c04_0003_rgb_1_red, nrom_cartridge_1_ppudata_out;
  wire [10:10] nrom_cartridge_1_vram_a10;
  wire [23:0] videodumper_rgb_1_addr;
  wire [31:0] videodumper_rgb_1_data;

  Clock CLK (.out(CLK_out));
  Pull_Resistor #(.pull(1)) pull_resistor_1 (.node(pull_resistor_1_node));
  _2C04_0003_RGB u_2c04_0003_rgb_1 (
    .SYNC(n2c04_0003_rgb_1_sync), .BLUE(n2c04_0003_rgb_1_blue), .GREEN(n2c04_0003_rgb_1_green),
    .RED(n2c04_0003_rgb_1_red), .nRES(nRES), .nINT(pull_resistor_1_node), .nDBE(nDBE), .RS2(RS[2]),
    .RS1(RS[1]), .RS0(RS[0]), .R_W(R_W), .D7(DB[7]), .D6(DB[6]), .D5(DB[5]), .D4(DB[4]), .D3(DB[3]),
    .D2(DB[2]), .D1(DB[1]), .D0(DB[0]), .nWR(n2c04_0003_rgb_1_nwr), .nRD(n2c04_0003_rgb_1_nrd),
    .PA13(n2c04_0003_rgb_1_pa8[5]), .PA12(n2c04_0003_rgb_1_pa8[4]), .PA11(n2c04_0003_rgb_1_pa8[3]),
    .PA10(n2c04_0003_rgb_1_pa8[2]), .PA9(n2c04_0003_rgb_1_pa8[1]), .PA8(n2c04_0003_rgb_1_pa8[0]),
    .PA7(n2c04_0003_rgb_1_pa0[7]), .PA6(n2c04_0003_rgb_1_pa0[6]), .PA5(n2c04_0003_rgb_1_pa0[5]),
    .PA4(n2c04_0003_rgb_1_pa0[4]), .PA3(n2c04_0003_rgb_1_pa0[3]), .PA2(n2c04_0003_rgb_1_pa0[2]),
    .PA1(n2c04_0003_rgb_1_pa0[1]), .PA0(n2c04_0003_rgb_1_pa0[0]), .ALE(n2c04_0003_rgb_1_ale),
    .PD7(nrom_cartridge_1_ppudata_out[7]), .PD6(nrom_cartridge_1_ppudata_out[6]),
    .PD5(nrom_cartridge_1_ppudata_out[5]), .PD4(nrom_cartridge_1_ppudata_out[4]),
    .PD3(nrom_cartridge_1_ppudata_out[3]), .PD2(nrom_cartridge_1_ppudata_out[2]),
    .PD1(nrom_cartridge_1_ppudata_out[1]), .PD0(nrom_cartridge_1_ppudata_out[0]),
    .PD7_W(n2c04_0003_rgb_1_pd0_w[7]), .PD6_W(n2c04_0003_rgb_1_pd0_w[6]), .PD5_W(n2c04_0003_rgb_1_pd0_w[5]),
    .PD4_W(n2c04_0003_rgb_1_pd0_w[4]), .PD3_W(n2c04_0003_rgb_1_pd0_w[3]), .PD2_W(n2c04_0003_rgb_1_pd0_w[2]),
    .PD1_W(n2c04_0003_rgb_1_pd0_w[1]), .PD0_W(n2c04_0003_rgb_1_pd0_w[0]), .CLK(CLK_out));  // open: D7_2, D6_2, D5_2, D4_2, D3_2, D2_2, D1_2, D0_2, AGND
  not not_1 (not_1_out, pull_resistor_1_node);
  LED led_1 (.in(not_1_out));
  VideoDumper_RGB videodumper_rgb_1 (
    .CLK(CLK_out), .RED(n2c04_0003_rgb_1_red), .GREEN(n2c04_0003_rgb_1_green), .BLUE(n2c04_0003_rgb_1_blue),
    .nSYNC(n2c04_0003_rgb_1_sync), .ADDR(videodumper_rgb_1_addr), .DATA(videodumper_rgb_1_data));
  LS373 ls373_1 (.LE(n2c04_0003_rgb_1_ale), .nOE(1'b0), .val_in(n2c04_0003_rgb_1_pa0), .val_out(ls373_1_val_out));
  RAM #(.addrWidth(24), .dataWidth(32), .bus("asynch")) ram_1 (
    .addr(videodumper_rgb_1_addr), .data(videodumper_rgb_1_data), .sel(1'b1), .ld(1'b0), .clr(1'b0));
  NROM_Cartridge nrom_cartridge_1 (
    .PPUData_In(n2c04_0003_rgb_1_pd0_w), .nRD(n2c04_0003_rgb_1_nrd), .nWR(n2c04_0003_rgb_1_nwr),
    .PPUAddr({n2c04_0003_rgb_1_pa8, ls373_1_val_out}), .nPA13(not_2_out),
    .PPUData_Out(nrom_cartridge_1_ppudata_out), .nVRAM_CS(nrom_cartridge_1_nvram_cs),
    .VRAM_A10(nrom_cartridge_1_vram_a10[10]), .V_Mirroring(1'b1));
  not not_2 (not_2_out, n2c04_0003_rgb_1_pa8[5]);
  SRAM sram_1 (
    .nCS(nrom_cartridge_1_nvram_cs), .nWE(n2c04_0003_rgb_1_nwr), .nOE(n2c04_0003_rgb_1_nrd),
    .Addr({nrom_cartridge_1_vram_a10[10], n2c04_0003_rgb_1_pa8[1:0], ls373_1_val_out}),
    .Data_In(n2c04_0003_rgb_1_pd0_w), .Data_Out(nrom_cartridge_1_ppudata_out));

  // Notes on the sheet:
  //   /SYNC actually
  //   PA0-7
  //   PPU Data Out
  //   PPU Data In
endmodule

module SRAM (
  input  nCS,
  input  nWE,
  input  nOE,
  input  [10:0] Addr,
  input  [7:0] Data_In,
  output [7:0] Data_Out
);

  wire not_1_out, not_2_out, not_3_out;

  not not_1 (not_1_out, nCS);
  not not_2 (not_2_out, nWE);
  not not_3 (not_3_out, nOE);
  RAM #(.addrWidth(11), .bus("separate")) ram_1 (
    .addr(Addr), .din(Data_In), .data(Data_Out), .str(not_2_out), .sel(not_1_out), .clk(not_1_out),
    .ld(not_3_out));  // open: clr
endmodule

module LS373 (
  input  LE,
  input  nOE,
  input  [7:0] val_in,
  output [7:0] val_out
);

  wire not_1_out;
  wire [7:0] register_1_q;

  not not_1 (not_1_out, nOE);
  Register #(.trigger("high")) register_1 (.D(val_in), .en(LE), .Q(register_1_q), .clk(LE));  // open: clr
  assign val_out = not_1_out ? register_1_q : 8'bz;  // Controlled_Buffer controlled_buffer_1
endmodule

module NROM_Cartridge (
  input  [7:0] PPUData_In,
  input  nRD,
  input  nWR,
  input  [13:0] PPUAddr,
  input  nPA13,
  input  V_Mirroring,
  output [7:0] PPUData_Out,
  output nVRAM_CS,
  output VRAM_A10
);

  wire nor_1_out;

  nor nor_1 (nor_1_out, nRD, PPUAddr[13]);
  ROM #(.addrWidth(13)) rom_1 (.addr(PPUAddr[12:0]), .data(PPUData_Out), .sel(nor_1_out));
  Multiplexer #(.enable("false")) multiplexer_1 (
    .in0(PPUAddr[11]), .in1(PPUAddr[10]), .out(VRAM_A10), .sel(V_Mirroring));

  assign nVRAM_CS = nPA13;

  // Notes on the sheet:
  //   N.C.
  //   N.C.
  //   1: V-Mirroring, 0: H-Mirroring
  //   Simple NROM cartridge (without PRG)
  //   contents of rom_1 (hex, n*v repeats v):
  //   3 f 1f 1f 1c 24 26 66 4*0 1f 3f 3f 7f e0 c0 80 fc 80 c0 0 20 0 20 60 0 f0 fc fe fe 60 70 18 7 f 1f
  //   3f 7f 7f 7f 1f 7 0 1e 3f 7f fc 7c 0 0 e0 f0 f8 f8 fc fc f8 c0 c2 67 2f 37 7f 7f ff ff 7 7 f f 7f 7e
  //   fc f0 f8 f8 f0 70 fd fe b4 f8 f8 f9 fb ff 37 36 5c 0 0 1 3 1f 1f 3f ff ff fc 70 70 38 8 24 e3 f0 f8
  //   70 70 38 ff ff ff 1f 4*0 4*1f 6*0 1 7 f f e 12 6*0 f 1f 0 0 f0 e0 c0 fe 40 60 0 0 0 10 30 0 f8 fe 13
  //   33 30 18 4 f 1f 1f 1f 3f 3f 1f 7 8 17 17 0 10 7e 3e 0 0 c0 e0 ff ff fe fe fc e0 40 a0 3f 3f 3f 5*1f
  //   37 27 23 3 1 0 0 0 f0 f0 f0 5*f8 cc 4*ff 70 0 8 ff ff ff fe f0 c0 80 0 5*f0 c0 80 0 fc fc f8 78 78
  //   78 7e 7e 10 60 80 0 78 78 7e 7e 0 3 f 1f 1f 1c 24 26 5*0 1f 3f 3f 0 e0 c0 80 fc 80 c0 0 0 0 20 60 0
  //   f0 fc fe 66 60 30 18 f 1f 3f 3f 7f 7f 3f 1f 0 16 2f 2f 20 fc 7c 0 0 e0 e0 f0 fe fc fc f8 c0 60 20 30
  //   7*3f 1f 2f 2f 2f f 7 3 0 0 f0 90 0 8 c 1c fc f8 10 4*f0 e0 c0 e0 f f 7 7 7 f f 3 1 3 1 4 7 f f 3 f8
  //   f0 e0 f0 b0 80 e0 e0 f8 f0 e0 70 b0 80 e0 e0 3 3f 7f 19 9 9 28 5c 0 30 70 7f ff ff f7 f3 f8 e0 e0 fc
  //   26 30 80 10 0 18 10 0 f8 f8 fe ff 3e 1e 3f 38 30 30 0 3a e7 f f 1f 1f 1f f 7 78 1e 80 fe 7e 7e 7f 7f
  //   ff fe fc c6 8e ee ff ff 3c 3f 1f f 7 3f 21 20 3 0 0 e 7 3f 3f 3f ff ff ff fe fe fe fc 70 ff 7f 3f e
  //   c0 c0 e0 e0 f 9f cf ff 7f 3f 1e e 0 80 c8 fe 7f 3f 1e e 20 c0 80 80 4*0 e0 9*0 3 f 1f 1f 1c 24 6*0
  //   1f 3f 0 4 e6 e0 ff ff 8f 83 e 4*1f 3 ff ff 26 26 60 78 18 f 7f ff 3f 3f 7f 7f 1f 0 7e ff 1 21 fe 7a
  //   6 fe fc fc ff ff fe fe fe de 5c 6c ff cf 87 7 7 f 1f 1f ff ff fe fc f8 b0 60 0 f8 f8 f0 b8 f8 f9 fb
  //   ff 28 30 18 40 0 1 3 f 1f 4*ff fe c0 80 10 ec e3 e0 e0 e0 c0 80 ff ff ff 3f 4*0 4*f 4*0 13 33 30 18
  //   4 f 1f 1f 1f 3f 3f 1f 7 9 13 17 0 10 7e 30 e0 f0 f0 e0 ff ff fe ff fe fc f8 e0 1f 1f f f f 1f 1f 1f
  //   17 17 3 5*0 f0 f0 f8 f8 b8 f8 f8 f8 d0 90 18 8 40 0 0 0 3f ff ff ff f6 c6 84 0 30 f0 f0 f1 f6 c6 84
  //   0 f0 e0 80 13*0 1f 1f 3f 3f 1f f f 1f 1f 1f 3f 3e 7c 78 f0 e0 f0 f0 f8 f8 b8 f8 f8 f0 b0 90 18 8 40
  //   0 0 0 e0 5*f0 f8 f0 c0 e0 fc fe ff 7f 3 0 1f 1f 1f 3f 3e 3c 38 18 0 0 10 38 3e 3c 38 18 0 3 7 7 a b
  //   c 4*0 7 f f f 3 0 e0 fc 20 20 10 3c 4*0 f0 fc fe fc f8 7 7 7 1f 1f 3e 21 1 7 f 1b 18 10 30 21 1 e0
  //   e0 e0 f0 f0 e0 c0 e0 a8 fc f8 0 0 0 c0 e0 7 f e 14 16 18 0 3f 0 0 f 1f 1f 1f 7 3c c0 f8 40 40 20 78
  //   0 c0 0 0 e0 f8 fc f8 f0 c0 3f e f 1f 3f 7c 70 38 fc ed c0 0 0 60 70 38 f0 f8 e4 fc fc 7c 0 0 7e 1e 4
  //   c c c 0 0 7 f e 14 16 18 0 f 0 0 f 1f 1f 1f 7 d 1f 1f 1f 1c c 7 7 7 1e 1c 1e f 7 0 7 7 e0 60 f0 70
  //   e0 e0 f0 80 60 90 0 80 0 e0 f0 80 7 1f 3f 12 13 8 1f 31 0 10 3f 7f 7f 3f 3 f c0 f0 40 0 30 18 c0 f8
  //   0 0 e0 f8 fc f8 b0 38 31 39 1f 1f f 5f 7e 3c 1f 7 0 e f 53 7c 3c f8 f8 f0 e0 e0 c0 0 0 f8 f8 f0 0 0
  //   80 0 0 0 e0 fc 27 27 11 3e 4 7 7 3 f7 ff ff fe fc 3f 7f 3f f 1f 3f 7f 4f 3e 7f ff e2 50 38 70 40 f8
  //   f9 f9 b7 ff ff e0 0 e8 71 1 4b 3 3 0 0 7 7 f 3f 3f 3f 26 4 5 3 1 30 30 30 26 4 f0 f0 f0 e0 c0 0 0 0
  //   fe fc e0 5*0 7 7 f 1f 3f f 1c 18 5 3 1 10 30 c 1c 18 4*e0 c0 80 0 0 c0 e0 f0 78 18 8 0 0 7 f 1f f 3f
  //   f 1c 18 7 f 3e 7c 30 c 1c 18 e0 e0 e0 40 c0 80 0 0 60 60 60 80 4*0 7f ff ff fb f f f 1f 73 f3 f0 f4
  //   f0 f0 70 60 3f 7e 7c 7c 3c 3c fc fc 4*0 3c 3c fc fc 60 70 18 8 f 1f 3f 7f 7f 7f 1f 7 b 1b 3b 7b fc
  //   7c 0 20 f0 f8 fc fe fc fc f8 e0 d0 d8 dc de b f 1f 1e 3c 3c 3c 7c c4 e0 e0 40 0 3c 3c 7c 1f 3f d 7 f
  //   e 1c 3c 1d 3c 3a 38 30 0 1c 3c 8*0 22 5*55 77 22 0 7 1f ff 7 1f f 6 8*0 3f 5*ff fb 76 0 0 cf 7 7f 0
  //   0 0 20 f8 ff c3 fd fe f0 40 0 0 3c fc fe e0 0 0 40 e0 40 40 41 41 4f 47 40 e0 40 3f 3e 3e 30 38 6*0
  //   e0 c0 0 0 0 f8 f8 f8 18 38 43 46 44 5*40 3c 39 3b 3f 4*0 80 c0 40 5*0 78 38 b8 f8 4*0 31 30 38 7c 7f
  //   ff ff fb 3f 3f f 77 77 f7 f7 f7 10 7e 3e 0 1e fe ff ff ff fe fe fe fa fa f3 e7 ff ff e3 c3 87 48 3c
  //   fc f0 f8 fc 7c 78 38 3c fc 0 ff c3 83 83 4*ff 0 c3 81 81 c3 ff 0 1f 1f f 7 1 11*0 f0 fb ff ff fe 3e
  //   c 4 0 b 1f 1f 1e 3e c 4 1f 1f f f 7 11*0 fb 4*ff 0 0 0 3 4*f 4*0 18 3c 7e 6e df df df 0 18 3c 7e 76
  //   fb fb fb 0 18 18 4*3c 1c 0 10 10 5*20 0 6*8 0 0 7*8 0 8 8 5*4 0 10 10 5*38 3c 7e 77 fb 9f 5f 8e 20 0
  //   18 3c e e 4 0 0 5c 2e 8f 3f 7b 77 7e 3c 0 0 4 6 1e 3c 18 0 13 4f 3f bf 3f 7a f8 f8 0 0 1 a 17 f 2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
  //   CHR-ROM (0x2000 bytes)
endmodule

module VideoDumper (
  input  CLK,
  input  [10:0] VIDEO_IN,
  output [23:0] ADDR,
  output [31:0] DATA
);

  wire counter_2_q, counter_3_q;
  wire [31:0] multiplexer_1_out, multiplexer_2_out, multiplexer_3_out, multiplexer_4_out, multiplexer_5_out,
       multiplexer_6_out, multiplexer_7_out, multiplexer_8_out, multiplexer_9_out, multiplexer_10_out,
       multiplexer_11_out, multiplexer_12_out, multiplexer_13_out, multiplexer_14_out, multiplexer_15_out,
       multiplexer_16_out, multiplexer_17_out, multiplexer_18_out, multiplexer_19_out, multiplexer_20_out;

  Multiplexer #(.width(32), .enable("false")) multiplexer_1 (
    .in0(32'h40400000), .in1(32'h400f3b64), .out(multiplexer_1_out), .sel(VIDEO_IN[10]));
  Multiplexer #(.width(32), .enable("false")) multiplexer_2 (
    .in0(32'h402f8d50), .in1(32'h4002f638), .out(multiplexer_2_out), .sel(VIDEO_IN[10]));
  Multiplexer #(.width(32), .enable("false")) multiplexer_3 (
    .in0(multiplexer_1_out), .in1(multiplexer_2_out), .out(multiplexer_3_out), .sel(VIDEO_IN[9]));
  Multiplexer #(.width(32), .enable("false")) multiplexer_4 (
    .in0(32'h40152f1b), .in1(32'h3fde9521), .out(multiplexer_4_out), .sel(VIDEO_IN[10]));
  Multiplexer #(.width(32), .enable("false")) multiplexer_5 (
    .in0(multiplexer_3_out), .in1(multiplexer_4_out), .out(multiplexer_5_out), .sel(VIDEO_IN[8]));
  Multiplexer #(.width(32), .enable("false")) multiplexer_6 (
    .in0(32'h40125e35), .in1(32'h3fda618d), .out(multiplexer_6_out), .sel(VIDEO_IN[10]));
  Multiplexer #(.width(32), .enable("false")) multiplexer_7 (
    .in0(multiplexer_5_out), .in1(multiplexer_6_out), .out(multiplexer_7_out), .sel(VIDEO_IN[7]));
  Multiplexer #(.width(32), .enable("false")) multiplexer_8 (
    .in0(32'h3ff00000), .in1(32'h3fb30a3d), .out(multiplexer_8_out), .sel(VIDEO_IN[10]));
  Counter #(.width(23), .max('h7fffff)) counter_1 (.Q(ADDR[23:1]), .clk(CLK));  // open: load, D, count, carry, clr
  Counter #(.width(1), .max('h1)) counter_2 (.Q(counter_2_q), .clk(CLK));  // open: load, D, count, carry, clr
  Counter #(.width(1), .max('h1), .trigger("falling")) counter_3 (
    .Q(counter_3_q), .clk(CLK));  // open: load, D, count, carry, clr
  Multiplexer #(.width(32), .enable("false")) multiplexer_9 (
    .in0(multiplexer_7_out), .in1(multiplexer_8_out), .out(multiplexer_9_out), .sel(VIDEO_IN[6]));
  Multiplexer #(.width(32), .enable("false")) multiplexer_10 (
    .in0(multiplexer_9_out), .in1(multiplexer_11_out), .out(multiplexer_10_out), .sel(VIDEO_IN[5]));
  Multiplexer #(.width(32), .enable("false")) multiplexer_11 (
    .in0(32'h3fdf1aa0), .in1(32'h3fa66f82), .out(multiplexer_11_out), .sel(VIDEO_IN[10]));
  xnor xnor_1 (ADDR[0], counter_2_q, counter_3_q);
  Multiplexer #(.width(32), .enable("false")) multiplexer_12 (
    .in0(multiplexer_10_out), .in1(multiplexer_13_out), .out(multiplexer_12_out), .sel(VIDEO_IN[4]));
  Multiplexer #(.width(32), .enable("false")) multiplexer_13 (
    .in0(32'h3fdb22d1), .in1(32'h3fa379b7), .out(multiplexer_13_out), .sel(VIDEO_IN[10]));
  Multiplexer #(.width(32), .enable("false")) multiplexer_14 (
    .in0(multiplexer_12_out), .in1(multiplexer_15_out), .out(multiplexer_14_out), .sel(VIDEO_IN[3]));
  Multiplexer #(.width(32), .enable("false")) multiplexer_15 (
    .in0(32'h3fa66666), .in1(32'h3f7844d0), .out(multiplexer_15_out), .sel(VIDEO_IN[10]));
  Multiplexer #(.width(32), .enable("false")) multiplexer_16 (
    .in0(32'h3f90c49c), .in1(32'h3f57fe6d), .out(multiplexer_16_out), .sel(VIDEO_IN[10]));
  Multiplexer #(.width(32), .enable("false")) multiplexer_17 (
    .in0(multiplexer_14_out), .in1(multiplexer_16_out), .out(multiplexer_17_out), .sel(VIDEO_IN[2]));
  Multiplexer #(.width(32), .enable("false")) multiplexer_18 (
    .in0(32'h3f800000), .in1(32'h3f3ef9db), .out(multiplexer_18_out), .sel(VIDEO_IN[10]));
  Multiplexer #(.width(32), .enable("false")) multiplexer_19 (
    .in0(multiplexer_17_out), .in1(multiplexer_18_out), .out(multiplexer_19_out), .sel(VIDEO_IN[1]));
  Multiplexer #(.width(32), .enable("false")) multiplexer_20 (
    .in0(32'h3f47ef9e), .in1(32'h3f1526fa), .out(multiplexer_20_out), .sel(VIDEO_IN[10]));
  Multiplexer #(.width(32), .enable("false")) multiplexer_21 (
    .in0(multiplexer_19_out), .in1(multiplexer_20_out), .out(DATA), .sel(VIDEO_IN[0]));

  // Other names for the same wires on the sheet: L0 = VIDEO_IN[0]; L1 = VIDEO_IN[1]; L2 = VIDEO_IN[2];
  //   L3 = VIDEO_IN[3]; L4 = VIDEO_IN[4]; L5 = VIDEO_IN[5]; L6 = VIDEO_IN[6]; L7 = VIDEO_IN[7]; L8 = VIDEO_IN[8];
  //   L9 = VIDEO_IN[9]; TINT = VIDEO_IN[10]

  // Notes on the sheet:
  //   White Level
  //   The invention of the org to make the ADDR tick EVERY half cycle.
endmodule

module VideoDumper_RGB (
  input  CLK,
  input  [7:0] RED,
  input  [7:0] GREEN,
  input  [7:0] BLUE,
  input  nSYNC,
  output [23:0] ADDR,
  output [31:0] DATA
);

  wire counter_2_q, counter_3_q;

  RGB_Decoder rgb_decoder_1 (.val(RED), .out_2(DATA[7:0]));
  RGB_Decoder rgb_decoder_2 (.val(GREEN), .out_2(DATA[15:8]));
  RGB_Decoder rgb_decoder_3 (.val(BLUE), .out_2(DATA[23:16]));
  assign DATA[31:24] = {{7{1'b0}}, nSYNC};  // Bit_Extender bit_extender_1
  Counter #(.width(23), .max('h7fffff)) counter_1 (.Q(ADDR[23:1]), .clk(CLK));  // open: load, D, count, carry, clr
  Counter #(.width(1), .max('h1)) counter_2 (.Q(counter_2_q), .clk(CLK));  // open: load, D, count, carry, clr
  Counter #(.width(1), .max('h1), .trigger("falling")) counter_3 (
    .Q(counter_3_q), .clk(CLK));  // open: load, D, count, carry, clr
  xnor xnor_1 (ADDR[0], counter_2_q, counter_3_q);

  // Notes on the sheet:
  //   The invention of the org to make the ADDR tick EVERY half cycle.
endmodule

module RGB_Decoder (
  input  [7:0] val,
  output [7:0] out_2
);

  wire not_1_out, priority_encoder_1_en_out;
  wire [2:0] multiplexer_1_out, priority_encoder_1_out;

  not not_1 (not_1_out, priority_encoder_1_en_out);
  Priority_Encoder priority_encoder_1 (
    .in0(val[0]), .in1(val[1]), .in2(val[2]), .in3(val[3]), .in4(val[4]), .in5(val[5]), .in6(val[6]),
    .in7(val[7]), .out(priority_encoder_1_out), .en_in(1'b1), .en_out(priority_encoder_1_en_out));  // open: gs
  Multiplexer #(.width(3), .enable("false")) multiplexer_1 (
    .in0(3'b000), .in1(priority_encoder_1_out), .out(multiplexer_1_out), .sel(not_1_out));
  Multiplier multiplier_1 (.a(8'h23), .b({{5{1'b0}}, multiplexer_1_out}), .out(out_2));  // open: cin, cout
endmodule
