// Logisim project Famicom_Evo.circ as structural Verilog: 13 circuits, main circuit Famicom
module Famicom (
);

  wire cartridge_port_n_vram_cs, cartridge_port_soundout, CLK_out, cpu_inst_m2, cpu_inst_n_in0,
       cpu_inst_n_in1, cpu_inst_rnw, fds_port_n_irq, fds_port_s4017_d1, fds_port_s4017_d2, fds_port_s4017_d3,
       fds_port_s4017_d4, Player_1_s4016_d0, Player_2_mic, Player_2_s4017_d0, ppu_inst_ale, ppu_inst_n_rd,
       ppu_inst_n_we, ppu_inst_video, pull_resistor_1_node, pull_resistor_2_node, pull_resistor_3_node,
       pull_resistor_10_node, RESET_SW_out, U7_TriStateArray_y5;
  wire [2:0] cpu_inst_out_0;
  wire [3:0] ppu_inst_ext_out, U3_DoubleDMX_n_y1, U3_DoubleDMX_n_y2;
  wire [7:0] cpu_inst_d_out, ppu_inst_ad_out, U4_vram_d_out, U7_TriStateArray_y1;
  wire [10:10] cartridge_port_vram_a10;
  wire [13:0] ppu_inst_ahi_out;
  wire [14:0] cpu_inst_a_out;
  wire [15:15] cpu_inst_a_out_2;

  Pull_Resistor #(.pull(1)) pull_resistor_1 (.node(pull_resistor_1_node));
  Clock CLK (.out(CLK_out));
  Pull_Resistor #(.pull(1)) pull_resistor_2 (.node(pull_resistor_2_node));
  P4 Player_1 (.OUT_0(cpu_inst_out_0[0]), .S4016_CUP(pull_resistor_1_node), .S4016_D0(Player_1_s4016_d0));
  P5 Player_2 (
    .OUT_0(cpu_inst_out_0[0]), .S4017_CUP(pull_resistor_2_node), .S4017_D0(Player_2_s4017_d0),
    .MIC(Player_2_mic));
  Pull_Resistor #(.pull(1)) pull_resistor_3 (.node(pull_resistor_3_node));
  P2 fds_port (
    .S4017_CUP(pull_resistor_2_node), .OUT_2(cpu_inst_out_0[2]), .OUT_1(cpu_inst_out_0[1]),
    .OUT_0(cpu_inst_out_0[0]), .S4016_CUP(pull_resistor_1_node), .SOUND(Player_2_mic),
    .n_IRQ(fds_port_n_irq), .S4017_D4(fds_port_s4017_d4), .S4017_D3(fds_port_s4017_d3),
    .S4017_D2(fds_port_s4017_d2), .S4017_D1(fds_port_s4017_d1), .S4017_D0(Player_2_s4017_d0),
    .S4016_D1(pull_resistor_3_node));
  Pull_Resistor #(.pull(1)) pull_resistor_4 (.node(Player_2_s4017_d0));
  Pull_Resistor #(.pull(1)) pull_resistor_5 (.node(fds_port_s4017_d2));
  Pull_Resistor #(.pull(1)) pull_resistor_6 (.node(fds_port_s4017_d4));
  Pull_Resistor #(.pull(1)) pull_resistor_7 (.node(Player_1_s4016_d0));
  Pull_Resistor #(.pull(1)) pull_resistor_8 (.node(fds_port_s4017_d3));
  Pull_Resistor #(.pull(1)) pull_resistor_9 (.node(fds_port_s4017_d1));
  U_40H368 U7_TriStateArray (
    .n_G1(cpu_inst_n_in0), .n_G2(1'b0), .A1(Player_1_s4016_d0), .A2(pull_resistor_3_node), .A3(cpu_inst_m2),
    .A4(Player_2_mic), .A5(ppu_inst_ahi_out[13]), .Y1(U7_TriStateArray_y1[0]), .Y2(U7_TriStateArray_y1[1]),
    .Y3(pull_resistor_1_node), .Y4(U7_TriStateArray_y1[2]), .Y5(U7_TriStateArray_y5));  // open: A6, Y6
  U_40H368 U8_TriStateArray (
    .n_G1(cpu_inst_n_in1), .n_G2(cpu_inst_n_in1), .A1(cpu_inst_m2), .A2(fds_port_s4017_d1),
    .A3(fds_port_s4017_d3), .A4(fds_port_s4017_d4), .A5(fds_port_s4017_d2), .A6(Player_2_s4017_d0),
    .Y1(pull_resistor_2_node), .Y2(U7_TriStateArray_y1[1]), .Y3(U7_TriStateArray_y1[3]),
    .Y4(U7_TriStateArray_y1[4]), .Y5(U7_TriStateArray_y1[2]), .Y6(U7_TriStateArray_y1[0]));
  Button #(.press("passive")) RESET_SW (.out(RESET_SW_out));
  APU cpu_inst (
    .CLK(CLK_out), .D_In(U7_TriStateArray_y1), .n_NMI(pull_resistor_10_node), .n_RST(RESET_SW_out),
    .n_IRQ(fds_port_n_irq), .DBG(1'b0), .D_Out(cpu_inst_d_out), .n_IN0(cpu_inst_n_in0),
    .n_IN1(cpu_inst_n_in1), .OUT_0(cpu_inst_out_0[0]), .OUT_1(cpu_inst_out_0[1]), .OUT_2(cpu_inst_out_0[2]),
    .AUX_A(Player_2_mic), .AUX_B(Player_2_mic), .M2(cpu_inst_m2),
    .A_Out({cpu_inst_a_out_2[15], cpu_inst_a_out}), .RnW(cpu_inst_rnw));
  S_RAM U1_wram (
    .n_CS(U3_DoubleDMX_n_y1[0]), .n_WE(cpu_inst_rnw), .n_OE(1'b0), .A_In(cpu_inst_a_out[10:0]),
    .D_In(U7_TriStateArray_y1), .D_Out(cpu_inst_d_out));
  Pull_Resistor #(.pull(1)) pull_resistor_10 (.node(pull_resistor_10_node));
  PPU ppu_inst (
    .CLK(CLK_out), .n_RST(1'b1), .RS0(cpu_inst_a_out[0]), .RS1(cpu_inst_a_out[1]), .RS2(cpu_inst_a_out[2]),
    .n_DBE(U3_DoubleDMX_n_y1[1]), .RnW(cpu_inst_rnw), .D_In(U7_TriStateArray_y1), .AD_In(U4_vram_d_out),
    .EXT_In(4'b0000), .ALE(ppu_inst_ale), .n_INT(pull_resistor_10_node), .n_RD(ppu_inst_n_rd),
    .n_WE(ppu_inst_n_we), .VIDEO(ppu_inst_video), .D_Out(cpu_inst_d_out), .AD_Out(ppu_inst_ad_out),
    .AHi_Out(ppu_inst_ahi_out[13:8]), .EXT_Out(ppu_inst_ext_out));
  // NoConnect on ppu_inst_ext_out
  S_RAM U4_vram (
    .n_CS(cartridge_port_n_vram_cs), .n_WE(ppu_inst_n_we), .n_OE(ppu_inst_n_rd),
    .A_In({cartridge_port_vram_a10[10], ppu_inst_ahi_out[9:0]}), .D_In(ppu_inst_ad_out), .D_Out(U4_vram_d_out));
  LS373 U2_Latch (.LE(ppu_inst_ale), .n_OE(1'b0), .D(ppu_inst_ad_out), .Q(ppu_inst_ahi_out[7:0]));
  LS139 U3_DoubleDMX (
    .n_EN1(U3_DoubleDMX_n_y2[1]), .n_EN2(1'b0), .A1_0(cpu_inst_a_out[13]), .A1_1(cpu_inst_a_out[14]),
    .A2_0(cpu_inst_m2), .A2_1(cpu_inst_a_out_2[15]), .n_Y1(U3_DoubleDMX_n_y1), .n_Y2(U3_DoubleDMX_n_y2));
  P3 tv_port (.AUDIO(cartridge_port_soundout), .VIDEO(ppu_inst_video));
  P1 cartridge_port (
    .A_In(cpu_inst_a_out), .M2(cpu_inst_m2), .PA_In(ppu_inst_ahi_out), .n_PA13(U7_TriStateArray_y5),
    .D_In(cpu_inst_d_out), .PD_In(ppu_inst_ad_out), .RnW(cpu_inst_rnw), .n_RD(ppu_inst_n_rd),
    .n_WE(ppu_inst_n_we), .n_ROMSEL(U3_DoubleDMX_n_y2[3]), .SoundIn(Player_2_mic),
    .SoundOut(cartridge_port_soundout), .n_IRQ(fds_port_n_irq), .VRAM_A10(cartridge_port_vram_a10[10]),
    .n_VRAM_CS(cartridge_port_n_vram_cs), .D_Out(U7_TriStateArray_y1), .PD_Out(U4_vram_d_out));
  Pull_Resistor #(.pull(1)) pull_resistor_11 (.node(fds_port_n_irq));

  // Notes on the sheet:
  //   These pull-up resistors in the original circuit are designated as RM1
  //   The A6/Y6 are used as an inverter for sound, but it makes no sense here.
  //   PA8-9
  //   WA0-10
  //   PA0-7 Latched
  //   /PA13
  //   VA0-10
  //   PA0-13
  //   A0-14
  //   PA0-7 Latched
  //   PA8-13
endmodule

module APU (
  input  CLK,
  input  [7:0] D_In,
  input  n_NMI,
  input  n_RST,
  input  n_IRQ,
  input  DBG,
  output [7:0] D_Out,
  output n_IN0,
  output n_IN1,
  output OUT_0,
  output OUT_1,
  output OUT_2,
  output AUX_A,
  output AUX_B,
  output M2,
  output [15:0] A_Out,
  output RnW
);
endmodule

module PPU (
  input  CLK,
  input  n_RST,
  input  RS0,
  input  RS1,
  input  RS2,
  input  n_DBE,
  input  RnW,
  input  [7:0] D_In,
  input  [7:0] AD_In,
  input  [3:0] EXT_In,
  output ALE,
  output n_INT,
  output n_RD,
  output n_WE,
  output VIDEO,
  output [7:0] D_Out,
  output [7:0] AD_Out,
  output [5:0] AHi_Out,
  output [3:0] EXT_Out
);
endmodule

module U_40H368 (
  input  n_G1,
  input  n_G2,
  input  A1,
  input  A2,
  input  A3,
  input  A4,
  input  A5,
  input  A6,
  output Y1,
  output Y2,
  output Y3,
  output Y4,
  output Y5,
  output Y6
);

  wire not_1_out, not_2_out;

  not not_1 (not_1_out, n_G1);
  not not_2 (not_2_out, n_G2);
  assign Y1 = not_1_out ? ~A1 : 1'bz;  // Controlled_Inverter controlled_inverter_1
  assign Y2 = not_1_out ? ~A2 : 1'bz;  // Controlled_Inverter controlled_inverter_2
  assign Y3 = not_1_out ? ~A3 : 1'bz;  // Controlled_Inverter controlled_inverter_3
  assign Y4 = not_1_out ? ~A4 : 1'bz;  // Controlled_Inverter controlled_inverter_4
  assign Y5 = not_2_out ? ~A5 : 1'bz;  // Controlled_Inverter controlled_inverter_5
  assign Y6 = not_2_out ? ~A6 : 1'bz;  // Controlled_Inverter controlled_inverter_6

  // Notes on the sheet:
  //   40H368
endmodule

module P1 (
  input  [14:0] A_In,
  input  M2,
  input  [13:0] PA_In,
  input  n_PA13,
  input  [7:0] D_In,
  input  [7:0] PD_In,
  input  RnW,
  input  n_RD,
  input  n_WE,
  input  n_ROMSEL,
  input  SoundIn,
  output SoundOut,
  output n_IRQ,
  output VRAM_A10,
  output n_VRAM_CS,
  output [7:0] D_Out,
  output [7:0] PD_Out
);
endmodule

module P2 (
  input  S4017_CUP,
  input  OUT_2,
  input  OUT_1,
  input  OUT_0,
  input  S4016_CUP,
  output SOUND,
  output n_IRQ,
  output S4017_D4,
  output S4017_D3,
  output S4017_D2,
  output S4017_D1,
  output S4017_D0,
  output S4016_D1
);
endmodule

module P3 (
  input  AUDIO,
  input  VIDEO
);
endmodule

module P4 (
  input  OUT_0,
  input  S4016_CUP,
  output S4016_D0
);
endmodule

module P5 (
  input  OUT_0,
  input  S4017_CUP,
  output S4017_D0,
  output MIC
);
endmodule

module LS139 (
  input  n_EN1,
  input  n_EN2,
  input  A1_0,
  input  A1_1,
  input  A2_0,
  input  A2_1,
  output [3:0] n_Y1,
  output [3:0] n_Y2
);

  wire nand_1_out, nand_2_out, nand_3_out, nand_4_out, nand_5_out, nand_6_out, nand_7_out, nand_8_out,
       not_1_out, not_2_out, not_3_out, not_4_out, not_5_out, not_6_out, not_7_out, not_8_out, not_9_out,
       not_10_out, not_11_out, not_12_out, not_13_out, not_14_out, not_15_out, not_16_out, not_17_out,
       not_18_out;

  not not_1 (not_1_out, n_EN1);
  not not_2 (not_2_out, n_EN2);
  not not_3 (not_3_out, A1_0);
  not not_4 (not_4_out, A1_1);
  not not_5 (not_5_out, A2_0);
  not not_6 (not_6_out, A2_1);
  not not_7 (not_7_out, not_3_out);
  not not_8 (not_8_out, not_4_out);
  not not_9 (not_9_out, not_5_out);
  not not_10 (not_10_out, not_6_out);
  nand nand_1 (nand_1_out, not_3_out, not_4_out, not_1_out);
  not not_11 (not_11_out, nand_1_out);
  nand nand_2 (nand_2_out, not_7_out, not_4_out, not_1_out);
  not not_12 (not_12_out, nand_2_out);
  nand nand_3 (nand_3_out, not_3_out, not_8_out, not_1_out);
  not not_13 (not_13_out, nand_3_out);
  nand nand_4 (nand_4_out, not_7_out, not_8_out, not_1_out);
  not not_14 (not_14_out, nand_4_out);
  nand nand_5 (nand_5_out, not_5_out, not_6_out, not_2_out);
  not not_15 (not_15_out, nand_5_out);
  nand nand_6 (nand_6_out, not_9_out, not_6_out, not_2_out);
  not not_16 (not_16_out, nand_6_out);
  nand nand_7 (nand_7_out, not_5_out, not_10_out, not_2_out);
  not not_17 (not_17_out, nand_7_out);
  nand nand_8 (nand_8_out, not_9_out, not_10_out, not_2_out);
  not not_18 (not_18_out, nand_8_out);
  not not_19 (n_Y1[0], not_11_out);
  not not_20 (n_Y1[1], not_12_out);
  not not_21 (n_Y1[2], not_13_out);
  not not_22 (n_Y1[3], not_14_out);
  not not_23 (n_Y2[0], not_15_out);
  not not_24 (n_Y2[1], not_16_out);
  not not_25 (n_Y2[2], not_17_out);
  not not_26 (n_Y2[3], not_18_out);

  // Notes on the sheet:
  //   Double inverting 2-DMX with #Enabler
endmodule

module LS373 (
  input  LE,
  input  n_OE,
  input  [7:0] D,
  output [7:0] Q
);

  wire not_1_out, not_2_out, not_3_out;
  wire [7:0] ls373_latch_1_q;

  not not_1 (not_1_out, LE);
  not not_2 (not_2_out, n_OE);
  not not_3 (not_3_out, not_1_out);
  LS373_Latch ls373_latch_1 (.LE(not_3_out), .n_LE(not_1_out), .D(D[0]), .Q(ls373_latch_1_q[0]));
  LS373_Latch ls373_latch_2 (.LE(not_3_out), .n_LE(not_1_out), .D(D[1]), .Q(ls373_latch_1_q[1]));
  LS373_Latch ls373_latch_3 (.LE(not_3_out), .n_LE(not_1_out), .D(D[2]), .Q(ls373_latch_1_q[2]));
  LS373_Latch ls373_latch_4 (.LE(not_3_out), .n_LE(not_1_out), .D(D[3]), .Q(ls373_latch_1_q[3]));
  LS373_Latch ls373_latch_5 (.LE(not_3_out), .n_LE(not_1_out), .D(D[4]), .Q(ls373_latch_1_q[4]));
  LS373_Latch ls373_latch_6 (.LE(not_3_out), .n_LE(not_1_out), .D(D[5]), .Q(ls373_latch_1_q[5]));
  LS373_Latch ls373_latch_7 (.LE(not_3_out), .n_LE(not_1_out), .D(D[6]), .Q(ls373_latch_1_q[6]));
  LS373_Latch ls373_latch_8 (.LE(not_3_out), .n_LE(not_1_out), .D(D[7]), .Q(ls373_latch_1_q[7]));
  assign Q = not_2_out ? ls373_latch_1_q : 8'bz;  // Controlled_Buffer controlled_buffer_1

  // Notes on the sheet:
  //   Octal D-type transparent latch; 3-state
endmodule

module S_RAM (
  input  n_CS,
  input  n_WE,
  input  n_OE,
  input  [10:0] A_In,
  input  [7:0] D_In,
  output [7:0] D_Out
);
endmodule

module LS373_Latch (
  input  LE,
  input  n_LE,
  input  D,
  output Q
);

  wire not_2_out, transmission_1_p2, transmission_1_p3, transmission_1_p4, transmission_1_p7,
       transmission_2_p1, transmission_2_p6;

  // Transmission_Gate transmission_1: pin names not known; wires that end beside it: n_LE, transmission_1_p2, transmission_1_p3, transmission_1_p4, transmission_1_p2, transmission_1_p3, transmission_1_p7, transmission_1_p2, transmission_1_p3
  // Transmission_Gate transmission_2: pin names not known; wires that end beside it: transmission_2_p1, transmission_2_p1, transmission_1_p3, transmission_1_p2, transmission_1_p4, transmission_2_p6
  D_Flip_Flop #(.trigger("high")) d_ff_1 (.D(D), .clk(LE), .Q(Q));  // open: Qn, preset, reset
  not not_1 (transmission_1_p7, not_2_out);
  not not_2 (not_2_out, transmission_1_p4);
  not not_3 (transmission_2_p6, not_2_out);

  // Notes on the sheet:
  //   LE
  //   ~LE
  //   D
  //   Q
endmodule
