// Logisim project Mappers_Evo.circ as structural Verilog
module main (
  input  [7:0] PD_OutCart,
  input  n_VRAM_CS,
  input  VRAM_A10,
  output [7:0] PD_InCart,
  output n_RD,
  output n_WR,
  output [13:0] PA0_13,
  output n_PA13
);

  wire CLK_out, dummyppu_1_ale, dummyppu_1_n_int, dummyppu_1_video, ppu_player_1_n_dbe, ppu_player_1_rnw,
       ppu_player_1_rs0, ppu_player_1_rs1, ppu_player_1_rs2;
  wire [3:0] dummyppu_1_ext_out;
  wire [7:0] dummyppu_1_d_out, ppu_player_1_d_out;

  Clock CLK (.out(CLK_out));
  PPU_Player ppu_player_1 (
    .CLK(CLK_out), .RnW(ppu_player_1_rnw), .RS0(ppu_player_1_rs0), .RS1(ppu_player_1_rs1),
    .RS2(ppu_player_1_rs2), .n_DBE(ppu_player_1_n_dbe), .D_Out(ppu_player_1_d_out));
  LED led_1 (.in(dummyppu_1_n_int));
  DummyPPU dummyppu_1 (
    .CLK(CLK_out), .n_RES(1'b1), .RnW(ppu_player_1_rnw), .D_In(ppu_player_1_d_out), .RS0(ppu_player_1_rs0),
    .RS1(ppu_player_1_rs1), .RS2(ppu_player_1_rs2), .n_DBE(ppu_player_1_n_dbe), .EXT_In(4'b0000),
    .AD_In(PD_OutCart), .n_INT(dummyppu_1_n_int), .D_Out(dummyppu_1_d_out), .EXT_Out(dummyppu_1_ext_out),
    .n_RD(n_RD), .n_WR(n_WR), .ALE(dummyppu_1_ale), .AD_Out(PD_InCart), .A8_13(PA0_13[13:8]),
    .VIDEO(dummyppu_1_video));
  // NoConnect on dummyppu_1_d_out
  // NoConnect on dummyppu_1_ext_out
  S_RAM s_ram_1 (
    .n_CS(n_VRAM_CS), .n_WE(n_WR), .n_OE(n_RD), .A_In({VRAM_A10, PA0_13[9:0]}), .D_In(PD_InCart),
    .D_Out(PD_OutCart));
  LS373 ls373_1 (.LE(dummyppu_1_ale), .n_OE(1'b0), .D(PD_InCart), .Q(PA0_13[7:0]));
  SaveToFile savetofile_1 (.VIDEO(dummyppu_1_video));
  not not_1 (n_PA13, PA0_13[13]);

  // Notes on the sheet:
  //   PA8-9
  //   PA0-7 Latched
  //   PA8-13
endmodule

module PPU_Player (
  input  CLK,
  output RnW,
  output RS0,
  output RS1,
  output RS2,
  output n_DBE,
  output [7:0] D_Out
);
endmodule

module DummyPPU (
  input  CLK,
  input  n_RES,
  input  RnW,
  input  [7:0] D_In,
  input  RS0,
  input  RS1,
  input  RS2,
  input  n_DBE,
  input  [3:0] EXT_In,
  input  [7:0] AD_In,
  output n_INT,
  output [7:0] D_Out,
  output [3:0] EXT_Out,
  output n_RD,
  output n_WR,
  output ALE,
  output [7:0] AD_Out,
  output [5:0] A8_13,
  output VIDEO
);
endmodule

module SaveToFile (
  input  VIDEO
);
endmodule
