// Logisim project 2C02_PPU.circ as structural Verilog
module _2C02_PPU (
  input  nDBE,
  input  RS0,
  input  RS1,
  input  RS2,
  input  R_W,
  input  D7,
  input  D6,
  input  D5,
  input  D4,
  input  D3,
  input  D2,
  input  D1,
  input  D0,
  input  nRES,
  input  in_15,
  input  in_16,
  input  in_17,
  input  in_18,
  input  in_19,
  input  in_20,
  input  in_21,
  input  in_22,
  input  in_23,
  input  DB5,
  input  DB4,
  input  DB3,
  input  DB2,
  input  DB1,
  input  DB0,
  input  DB_PAR,
  input  TH_MUX,
  input  EXT3,
  input  EXT2,
  input  EXT1,
  input  EXT0,
  output D7_2,
  output D6_2,
  output D5_2,
  output D4_2,
  output D3_2,
  output D2_2,
  output D1_2,
  output D0_2,
  output nINT,
  output [10:0] VOUT,
  output nWR,
  output nRD,
  output A13,
  output A12,
  output A11,
  output A10,
  output A9,
  output A8
);

  wire CLK_out, color_buffer_bit_1_cb_ram, color_buffer_bit_1_db_2, color_buffer_bit_1_nout,
       color_buffer_bit_2_cb_ram, color_buffer_bit_2_db_2, color_buffer_bit_2_nout,
       color_buffer_bit_3_cb_ram, color_buffer_bit_3_db_2, color_buffer_bit_3_nout,
       color_buffer_bit_4_cb_ram, color_buffer_bit_4_db_2, color_buffer_bit_4_nout,
       color_buffer_bit_5_cb_ram, color_buffer_bit_5_db_2, color_buffer_bit_5_nout,
       color_buffer_bit_6_cb_ram, color_buffer_bit_6_db_2, color_buffer_bit_6_nout, color_control_1_cb_db,
       color_control_1_color_en, color_control_1_db_cb, color_ram_1_ram_cb0, color_ram_1_ram_cb1,
       color_ram_1_ram_cb2, color_ram_1_ram_cb3, color_ram_1_ram_cy0, color_ram_1_ram_cy1,
       control_unit_1__0_hpos, control_unit_1_blnk, control_unit_1_burst, control_unit_1_clip_b,
       control_unit_1_clip_o, control_unit_1_e_ev, control_unit_1_eval, control_unit_1_f_at,
       control_unit_1_f_nt, control_unit_1_f_ta, control_unit_1_f_tb, control_unit_1_hc,
       control_unit_1_i_oam2, control_unit_1_nfo, control_unit_1_nvis, control_unit_1_par_o,
       control_unit_1_picture, control_unit_1_s_ev, control_unit_1_sc_cnt, control_unit_1_sync,
       control_unit_1_vb, control_unit_1_vc, control_unit_1_vclr, control_unit_1_vin, control_unit_1_vset,
       cpu_data_pad_1_cpu_ppu, cpu_data_pad_2_cpu_ppu, cpu_data_pad_3_cpu_ppu, cpu_data_pad_4_cpu_ppu,
       cpu_data_pad_5_cpu_ppu, cpu_data_pad_6_cpu_ppu, cpu_data_pad_7_cpu_ppu, cpu_data_pad_8_cpu_ppu,
       h_counter_1_h0, h_counter_1_h1, h_counter_1_h2, h_counter_1_h3, h_counter_1_h4, h_counter_1_h5,
       h_counter_1_h6, h_counter_1_h7, h_counter_1_h8, hv_select_1__0, hv_select_1__0_1, hv_select_1__0_7a,
       hv_select_1__0_7b, hv_select_1__0_63, hv_select_1__0_255, hv_select_1__2_3, hv_select_1__4_5,
       hv_select_1__6_7, hv_select_1__63, hv_select_1__65, hv_select_1__240, hv_select_1__241,
       hv_select_1__241_2, hv_select_1__244, hv_select_1__247, hv_select_1__255, hv_select_1__256,
       hv_select_1__256_319, hv_select_1__261, hv_select_1__261_2, hv_select_1__261_3, hv_select_1__270,
       hv_select_1__279, hv_select_1__279_2, hv_select_1__304, hv_select_1__308, hv_select_1__323,
       hv_select_1__328, hv_select_1__335_339, hv_select_1__336_340a, hv_select_1__336_340b,
       hv_select_1__340, interrupt_control_1_db7, interrupt_control_1_int, pixel_clock_1_pclk,
       register_select_1_nr2, register_select_1_nr7, reset_ff_1_rc, reset_ff_1_res, rw_control_1_nrd,
       rw_control_1_nwr, undriven, undriven_2, undriven_3, undriven_4, undriven_5, undriven_6, undriven_7,
       undriven_8, v_counter_1_v0, v_counter_1_v1, v_counter_1_v2, v_counter_1_v3, v_counter_1_v4,
       v_counter_1_v5, v_counter_1_v6, v_counter_1_v7, v_counter_1_v8;

  Clock CLK (.out(CLK_out));
  COLOR_BUFFER_BIT color_buffer_bit_1 (
    .PCLK(pixel_clock_1_pclk), .CB_DB(color_control_1_cb_db), .DB_CB(color_control_1_db_cb), .DB(DB0),
    .RAM_CB(color_ram_1_ram_cb3), .OE(color_control_1_color_en), .DB_2(color_buffer_bit_1_db_2),
    .nout(color_buffer_bit_1_nout), .CB_RAM(color_buffer_bit_1_cb_ram));
  not not_1 (nINT, interrupt_control_1_int);
  INTERRUPT_CONTROL interrupt_control_1 (
    .VSET(control_unit_1_vset), .VCLR(control_unit_1_vclr), .nDBE(nDBE), .nR2(register_select_1_nr2),
    .VBL_EN(1'b1), .INT(interrupt_control_1_int), .DB7(interrupt_control_1_db7));
  COLOR_BUFFER_BIT color_buffer_bit_2 (
    .PCLK(pixel_clock_1_pclk), .CB_DB(color_control_1_cb_db), .DB_CB(color_control_1_db_cb), .DB(DB1),
    .RAM_CB(color_ram_1_ram_cb2), .OE(color_control_1_color_en), .DB_2(color_buffer_bit_2_db_2),
    .nout(color_buffer_bit_2_nout), .CB_RAM(color_buffer_bit_2_cb_ram));
  PIXEL_CLOCK pixel_clock_1 (.CLK(CLK_out), .RES(reset_ff_1_res), .PCLK(pixel_clock_1_pclk));
  RESET_FF reset_ff_1 (.nRES(nRES), .RESCL(control_unit_1_vclr), .RES(reset_ff_1_res), .RC(reset_ff_1_rc));
  COLOR_BUFFER_BIT color_buffer_bit_3 (
    .PCLK(pixel_clock_1_pclk), .CB_DB(color_control_1_cb_db), .DB_CB(color_control_1_db_cb), .DB(DB2),
    .RAM_CB(color_ram_1_ram_cb1), .OE(color_control_1_color_en), .DB_2(color_buffer_bit_3_db_2),
    .nout(color_buffer_bit_3_nout), .CB_RAM(color_buffer_bit_3_cb_ram));
  VIDEO_OUT video_out_1 (
    .CLK(CLK_out), .RES(reset_ff_1_res), .nTR(1'b1), .nTG(1'b1), .nTB(1'b1), .PCLK(pixel_clock_1_pclk),
    .nCC0(color_buffer_bit_4_nout), .nCC1(color_buffer_bit_3_nout), .nCC2(color_buffer_bit_2_nout),
    .nCC3(color_buffer_bit_1_nout), .SYNC(control_unit_1_sync), .BURST(control_unit_1_burst),
    .PICTURE(control_unit_1_picture), .nLL0(color_buffer_bit_6_nout), .nLL1(color_buffer_bit_5_nout),
    .out_16(VOUT));
  COLOR_BUFFER_BIT color_buffer_bit_4 (
    .PCLK(pixel_clock_1_pclk), .CB_DB(color_control_1_cb_db), .DB_CB(color_control_1_db_cb), .DB(DB3),
    .RAM_CB(color_ram_1_ram_cb0), .OE(color_control_1_color_en), .DB_2(color_buffer_bit_4_db_2),
    .nout(color_buffer_bit_4_nout), .CB_RAM(color_buffer_bit_4_cb_ram));
  COLOR_BUFFER_BIT color_buffer_bit_5 (
    .PCLK(pixel_clock_1_pclk), .CB_DB(color_control_1_cb_db), .DB_CB(color_control_1_db_cb), .DB(DB4),
    .RAM_CB(color_ram_1_ram_cy1), .OE(1'b1), .DB_2(color_buffer_bit_5_db_2), .nout(color_buffer_bit_5_nout),
    .CB_RAM(color_buffer_bit_5_cb_ram));
  COLOR_RAM color_ram_1 (
    .PAL2(in_21), .PAL3(in_20), .PCLK(pixel_clock_1_pclk), .PAL4(in_19), .PAL0(in_23), .PAL1(in_22),
    .CB3_RAM(color_buffer_bit_1_cb_ram), .RAM_CB3(color_ram_1_ram_cb3), .CB2_RAM(color_buffer_bit_2_cb_ram),
    .RAM_CB2(color_ram_1_ram_cb2), .CB1_RAM(color_buffer_bit_3_cb_ram), .RAM_CB1(color_ram_1_ram_cb1),
    .CB0_RAM(color_buffer_bit_4_cb_ram), .RAM_CB0(color_ram_1_ram_cb0), .CY1_RAM(color_buffer_bit_5_cb_ram),
    .RAM_CY1(color_ram_1_ram_cy1), .CY0_RAM(color_buffer_bit_6_cb_ram), .RAM_CY0(color_ram_1_ram_cy0));
  COLOR_CONTROL color_control_1 (
    .PCLK(pixel_clock_1_pclk), .DB_PAR(DB_PAR), .PICTURE(control_unit_1_picture), .BW(in_15),
    .TH_MUX(TH_MUX), .nR7(register_select_1_nr7), .nDBE(nDBE), .DB_CB(color_control_1_db_cb),
    .CB_DB(color_control_1_cb_db), .COLOR_EN(color_control_1_color_en));
  COLOR_BUFFER_BIT color_buffer_bit_6 (
    .PCLK(pixel_clock_1_pclk), .CB_DB(color_control_1_cb_db), .DB_CB(color_control_1_db_cb), .DB(DB5),
    .RAM_CB(color_ram_1_ram_cy0), .OE(1'b1), .DB_2(color_buffer_bit_6_db_2), .nout(color_buffer_bit_6_nout),
    .CB_RAM(color_buffer_bit_6_cb_ram));
  HV_SELECT hv_select_1 (
    .H8(h_counter_1_h8), .H7(h_counter_1_h7), .H6(h_counter_1_h6), .H5(h_counter_1_h5), .H4(h_counter_1_h4),
    .H3(h_counter_1_h3), .H2(h_counter_1_h2), .H1(h_counter_1_h1), .H0(h_counter_1_h0),
    .VB(control_unit_1_vb), .BLNK(control_unit_1_blnk), ._279(hv_select_1__279), ._256(hv_select_1__256),
    ._65(hv_select_1__65), ._0_7A(hv_select_1__0_7a), ._0_7B(hv_select_1__0_7b),
    ._335_339(hv_select_1__335_339), ._63(hv_select_1__63), ._255(hv_select_1__255),
    ._0_63(hv_select_1__0_63), ._256_319(hv_select_1__256_319), ._0_255(hv_select_1__0_255),
    ._0_1(hv_select_1__0_1), ._6_7(hv_select_1__6_7), ._4_5(hv_select_1__4_5),
    ._336_340A(hv_select_1__336_340a), ._336_340B(hv_select_1__336_340b), ._2_3(hv_select_1__2_3),
    ._270(hv_select_1__270), ._328(hv_select_1__328), ._279_2(hv_select_1__279_2), ._304(hv_select_1__304),
    ._323(hv_select_1__323), ._308(hv_select_1__308), ._340(hv_select_1__340), ._247(hv_select_1__247),
    .V8(v_counter_1_v8), .V7(v_counter_1_v7), .V6(v_counter_1_v6), .V5(v_counter_1_v5), .V4(v_counter_1_v4),
    .V3(v_counter_1_v3), .V2(v_counter_1_v2), .V1(v_counter_1_v1), .V0(v_counter_1_v0),
    ._244(hv_select_1__244), ._261(hv_select_1__261), ._241(hv_select_1__241), ._241_2(hv_select_1__241_2),
    ._0(hv_select_1__0), ._240(hv_select_1__240), ._261_2(hv_select_1__261_2), ._261_3(hv_select_1__261_3));
  H_COUNTER h_counter_1 (
    .HC(control_unit_1_hc), .RES(reset_ff_1_res), .CLK(pixel_clock_1_pclk), .H0(h_counter_1_h0),
    .H1(h_counter_1_h1), .H2(h_counter_1_h2), .H3(h_counter_1_h3), .H4(h_counter_1_h4), .H5(h_counter_1_h5),
    .H6(h_counter_1_h6), .H7(h_counter_1_h7), .H8(h_counter_1_h8));
  V_COUNTER v_counter_1 (
    .VC(control_unit_1_vc), .RES(reset_ff_1_res), .CLK(pixel_clock_1_pclk), .V0(v_counter_1_v0),
    .V1(v_counter_1_v1), .V2(v_counter_1_v2), .V3(v_counter_1_v3), .V4(v_counter_1_v4), .V5(v_counter_1_v5),
    .V6(v_counter_1_v6), .V7(v_counter_1_v7), .V8(v_counter_1_v8), .VIN(control_unit_1_vin));
  CONTROL_UNIT control_unit_1 (
    .PCLK(pixel_clock_1_pclk), .nOBCLIP(in_16), .nBGCLIP(in_17), .BLACK(in_18), ._279(hv_select_1__279),
    ._256(hv_select_1__256), ._65(hv_select_1__65), ._0_7A(hv_select_1__0_7a), ._0_7B(hv_select_1__0_7b),
    ._336_339(hv_select_1__335_339), ._63(hv_select_1__63), ._255(hv_select_1__255),
    ._0_63(hv_select_1__0_63), ._256_319(hv_select_1__256_319), ._0_255(hv_select_1__0_255),
    ._0_1(hv_select_1__0_1), ._6_7(hv_select_1__6_7), ._4_5(hv_select_1__4_5),
    ._336_340A(hv_select_1__336_340a), ._336_340B(hv_select_1__336_340b), ._2_3(hv_select_1__2_3),
    ._270(hv_select_1__270), ._328(hv_select_1__328), ._279_2(hv_select_1__279_2), ._304(hv_select_1__304),
    ._323(hv_select_1__323), ._308(hv_select_1__308), ._247(hv_select_1__247), ._244(hv_select_1__244),
    ._261(hv_select_1__261), ._241(hv_select_1__241), ._241_2(hv_select_1__241_2), ._0(hv_select_1__0),
    ._240(hv_select_1__240), ._261_2(hv_select_1__261_2), ._261_3(hv_select_1__261_3),
    .S_EV(control_unit_1_s_ev), .CLIP_O(control_unit_1_clip_o), .CLIP_B(control_unit_1_clip_b),
    ._0_HPOS(control_unit_1__0_hpos), .EVAL(control_unit_1_eval), .E_EV(control_unit_1_e_ev),
    .I_OAM2(control_unit_1_i_oam2), .PAR_O(control_unit_1_par_o), .nVIS(control_unit_1_nvis),
    .F_NT(control_unit_1_f_nt), .F_TB(control_unit_1_f_tb), .F_TA(control_unit_1_f_ta),
    .nFO(control_unit_1_nfo), .F_AT(control_unit_1_f_at), .SC_CNT(control_unit_1_sc_cnt),
    .SYNC(control_unit_1_sync), .BURST(control_unit_1_burst), .PICTURE(control_unit_1_picture),
    .VSET(control_unit_1_vset), .VB(control_unit_1_vb), .BLNK(control_unit_1_blnk),
    .VCLR(control_unit_1_vclr), ._340(hv_select_1__340), .RES(reset_ff_1_res), .V8(v_counter_1_v8),
    .VIN(control_unit_1_vin), .HC(control_unit_1_hc), .VC(control_unit_1_vc));
  MUX mux_1 ();  // open: PCLK, BGC0, BGC1, BGC2, BGC3, ZCOL0, ZCOL1, ZCOL2, ZCOL3, ZPRIO, EXT0_IN, EXT1_IN, EXT2_IN, EXT3_IN, THO0, THO1, THO2, THO3, THO4, TH_MUX, PAL0, PAL1, PAL2, PAL3, PAL4, EXT0_OUT, EXT1_OUT, EXT2_OUT, EXT3_OUT
  CONTROL_REGS control_regs_1 ();  // open: nDBE, nW0, RC, nW1, DB0, DB1, DB2, DB3, DB4, DB5, DB6, DB7, BW, I1_32, OBSEL, nBGCLIP, BGSEL, nOBCLIP, BGE, BLACK, O8_16, nSLAVE, OBE, VBL, nTR, nTG, nTB
  RW_CONTROL rw_control_1 (.R_W(R_W), .nDBE(nDBE), .nRD(rw_control_1_nrd), .nWR(rw_control_1_nwr));
  REGISTER_SELECT register_select_1 (
    .nDBE(nDBE), .RC(reset_ff_1_rc), .RS0(RS0), .RS1(RS1), .RS2(RS2), .R_W(R_W), .nR7(register_select_1_nr7),
    .nR2(register_select_1_nr2));  // open: nW6_1, nW6_2, nW5_1, nW5_2, nW7, nW4, nW3, nW1, nW0, nR4
  CPU_DATA_PAD cpu_data_pad_1 (
    .nRD(rw_control_1_nrd), .nWR(rw_control_1_nwr), .PPU_CPU(undriven), .CPU_PPU(cpu_data_pad_1_cpu_ppu),
    .PPU_data_out(D7_2), .PPU_data_in(D7));
  CPU_DATA_PAD cpu_data_pad_2 (
    .nRD(rw_control_1_nrd), .nWR(rw_control_1_nwr), .PPU_CPU(undriven_2), .CPU_PPU(cpu_data_pad_2_cpu_ppu),
    .PPU_data_out(D6_2), .PPU_data_in(D6));
  CPU_DATA_PAD cpu_data_pad_3 (
    .nRD(rw_control_1_nrd), .nWR(rw_control_1_nwr), .PPU_CPU(undriven_5), .CPU_PPU(cpu_data_pad_3_cpu_ppu),
    .PPU_data_out(D5_2), .PPU_data_in(D5));
  CPU_DATA_PAD cpu_data_pad_4 (
    .nRD(rw_control_1_nrd), .nWR(rw_control_1_nwr), .PPU_CPU(undriven_6), .CPU_PPU(cpu_data_pad_4_cpu_ppu),
    .PPU_data_out(D4_2), .PPU_data_in(D4));
  CPU_DATA_PAD cpu_data_pad_5 (
    .nRD(rw_control_1_nrd), .nWR(rw_control_1_nwr), .PPU_CPU(undriven_7), .CPU_PPU(cpu_data_pad_5_cpu_ppu),
    .PPU_data_out(D3_2), .PPU_data_in(D3));
  CPU_DATA_PAD cpu_data_pad_6 (
    .nRD(rw_control_1_nrd), .nWR(rw_control_1_nwr), .PPU_CPU(undriven_3), .CPU_PPU(cpu_data_pad_6_cpu_ppu),
    .PPU_data_out(D2_2), .PPU_data_in(D2));
  VRAM_BUS_CONTROL vram_bus_control_1 ();  // open: PCLK, H0, BLNK, nR7, nW7, nDBE, nPA8, nPA9, nPA10, nPA11, nPA12, WR, PD_RB, nALE, TSTEP, DB_PAR, RD, TH_MUX, XRB
  CPU_DATA_PAD cpu_data_pad_7 (
    .nRD(rw_control_1_nrd), .nWR(rw_control_1_nwr), .PPU_CPU(undriven_4), .CPU_PPU(cpu_data_pad_7_cpu_ppu),
    .PPU_data_out(D1_2), .PPU_data_in(D1));
  OAM_COUNTER oam_counter_1 ();  // open: POLY, LOAD, STEP, RES, D0, D1, D2, D3, D4, D5, D6, D7, out0, out1, out2, out3, out4, out5, out6, out7, COUT
  OAM_SUB oam_sub_1 ();  // open: PCLK, OB0, OB1, OB2, OB3, OB4, OB5, OB6, OB7, V0, V1, V2, V3, V4, V5, V6, V7, OV0, OV1, OV2, OV3, OV4, OV5, OV6, OV7
  CPU_DATA_PAD cpu_data_pad_8 (
    .nRD(rw_control_1_nrd), .nWR(rw_control_1_nwr), .PPU_CPU(undriven_8), .CPU_PPU(cpu_data_pad_8_cpu_ppu),
    .PPU_data_out(D0_2), .PPU_data_in(D0));
  OAM oam_1 ();  // open: PCLK, nOAM0, nOAM1, nOAM2, nOAM3, nOAM4, nOAM5, nOAM6, nOAM7, OAM8, OB0_OAM, OAM_OB0, OB1_OAM, OAM_OB1, OB2_OAM, OAM_OB2, OB3_OAM, OAM_OB3, OB4_OAM, OAM_OB4, OB5_OAM, OAM_OB5, OB6_OAM, OAM_OB6, OB7_OAM, OAM_OB7
  BG_COLOR bg_color_1 ();  // open: PCLK, PD0, PD1, PD2, PD3, PD4, PD5, PD6, PD7, CLPB, F_TA, F_TB, F_AT, nFO, H0, THO1, TVO1, FH0, FH1, FH2, BGC0, BGC1, BGC2, BGC3

  // Notes on the sheet:
  //   2C02 PPU
  //   VRAM INTERFACE
  //   PCLK
  //   MASTER/SLAVE
  //   CPU INTERFACE
  //   Logisim doesn't support bidirectional pads and wires
  //   So we have to add workaround by separate I/O wires
endmodule

module D_latch (
  input  EN,
  input  D,
  output Q,
  output NOT_Q
);

  D_Flip_Flop #(.trigger("high")) d_ff_1 (.clk(EN), .D(D), .Q(Q), .Qn(NOT_Q));  // open: preset, en, reset
endmodule

module PIXEL_CLOCK (
  input  CLK,
  input  RES,
  output PCLK
);

  wire d_latch_1_not_q, d_latch_2_not_q, d_latch_3_not_q, nor_1_out, not_1_out;

  not not_1 (not_1_out, CLK);
  nor nor_1 (nor_1_out, RES, PCLK);
  D_latch d_latch_1 (.EN(CLK), .D(nor_1_out), .NOT_Q(d_latch_1_not_q));  // open: Q
  D_latch d_latch_2 (.EN(not_1_out), .D(d_latch_1_not_q), .NOT_Q(d_latch_2_not_q));  // open: Q
  D_latch d_latch_3 (.EN(CLK), .D(d_latch_2_not_q), .NOT_Q(d_latch_3_not_q));  // open: Q
  D_latch d_latch_4 (.EN(not_1_out), .D(d_latch_3_not_q), .NOT_Q(PCLK));  // open: Q

  // Notes on the sheet:
  //   Pixel clock is disabled during RESET (PPU stall)
  //   PCLK = CLK / 4
endmodule

module RESET_FF (
  input  nRES,
  input  RESCL,
  output RES,
  output RC
);

  wire nor_1_out;

  not not_1 (RES, nRES);
  nor nor_1 (nor_1_out, RES, RC);
  nor nor_2 (RC, nor_1_out, RESCL);

  // Notes on the sheet:
  //   Reset flip/flop remains set after RESET, until not cleared by RESCL
  //   Reset flip/flop
  //   (REG CLEAR)
endmodule

module COUNTER_BIT (
  input  in,
  input  CLK,
  input  clear,
  input  RES,
  output value
);

  wire d_latch_1_q, multiplexer_1_out, multiplexer_2_out, nor_2_out, not_1_out, not_2_out;

  not not_1 (not_1_out, CLK);
  Multiplexer multiplexer_1 (.in0(not_2_out), .in1(value), .out(multiplexer_1_out), .sel(in));  // open: en
  not not_2 (not_2_out, multiplexer_2_out);
  Multiplexer multiplexer_2 (.in0(value), .in1(nor_2_out), .out(multiplexer_2_out), .sel(CLK));  // open: en
  nor nor_1 (value, not_2_out, RES);
  nor nor_2 (nor_2_out, d_latch_1_q, clear);
  D_latch d_latch_1 (.EN(not_1_out), .D(multiplexer_1_out), .Q(d_latch_1_q));  // open: NOT_Q

  // Notes on the sheet:
  //   carry_in
  //   clear manually
  //   global RESET
  //   carry_out
endmodule

module H_COUNTER (
  input  HC,
  input  RES,
  input  CLK,
  output H0,
  output H1,
  output H2,
  output H3,
  output H4,
  output H5,
  output H6,
  output H7,
  output H8
);

  wire and_1_out, and_2_out, and_3_out, and_4_out, and_5_out, and_6_out, and_7_out, and_8_out;

  COUNTER_BIT counter_bit_1 (.in(1'b1), .CLK(CLK), .clear(HC), .RES(RES), .value(H0));
  and and_1 (and_1_out, H0, 1'b1);
  COUNTER_BIT counter_bit_2 (.in(and_1_out), .CLK(CLK), .clear(HC), .RES(RES), .value(H1));
  and and_2 (and_2_out, H1, and_1_out);
  COUNTER_BIT counter_bit_3 (.in(and_2_out), .CLK(CLK), .clear(HC), .RES(RES), .value(H2));
  and and_3 (and_3_out, H2, and_2_out);
  COUNTER_BIT counter_bit_4 (.in(and_3_out), .CLK(CLK), .clear(HC), .RES(RES), .value(H3));
  and and_4 (and_4_out, H3, and_3_out);
  COUNTER_BIT counter_bit_5 (.in(and_4_out), .CLK(CLK), .clear(HC), .RES(RES), .value(H4));
  and and_5 (and_5_out, H4, H3, H2, H1, H0);
  COUNTER_BIT counter_bit_6 (.in(and_5_out), .CLK(CLK), .clear(HC), .RES(RES), .value(H5));
  and and_6 (and_6_out, H5, and_5_out);
  COUNTER_BIT counter_bit_7 (.in(and_6_out), .CLK(CLK), .clear(HC), .RES(RES), .value(H6));
  and and_7 (and_7_out, H6, and_6_out);
  COUNTER_BIT counter_bit_8 (.in(and_7_out), .CLK(CLK), .clear(HC), .RES(RES), .value(H7));
  and and_8 (and_8_out, H7, and_7_out);
  COUNTER_BIT counter_bit_9 (.in(and_8_out), .CLK(CLK), .clear(HC), .RES(RES), .value(H8));

  // Notes on the sheet:
  //   reduce propagation delay
endmodule

module V_COUNTER (
  input  VC,
  input  RES,
  input  CLK,
  input  VIN,
  output V0,
  output V1,
  output V2,
  output V3,
  output V4,
  output V5,
  output V6,
  output V7,
  output V8
);

  wire and_1_out, and_2_out, and_3_out, and_4_out, and_5_out, and_6_out, and_7_out, and_8_out;

  COUNTER_BIT counter_bit_1 (.in(VIN), .CLK(CLK), .clear(VC), .RES(RES), .value(V0));
  and and_1 (and_1_out, V0, VIN);
  COUNTER_BIT counter_bit_2 (.in(and_1_out), .CLK(CLK), .clear(VC), .RES(RES), .value(V1));
  and and_2 (and_2_out, V1, and_1_out);
  COUNTER_BIT counter_bit_3 (.in(and_2_out), .CLK(CLK), .clear(VC), .RES(RES), .value(V2));
  and and_3 (and_3_out, V2, and_2_out);
  COUNTER_BIT counter_bit_4 (.in(and_3_out), .CLK(CLK), .clear(VC), .RES(RES), .value(V3));
  and and_4 (and_4_out, V3, and_3_out);
  COUNTER_BIT counter_bit_5 (.in(and_4_out), .CLK(CLK), .clear(VC), .RES(RES), .value(V4));
  and and_5 (and_5_out, V4, V3, V2, V1, V0);
  COUNTER_BIT counter_bit_6 (.in(and_5_out), .CLK(CLK), .clear(VC), .RES(RES), .value(V5));
  and and_6 (and_6_out, V5, and_5_out);
  COUNTER_BIT counter_bit_7 (.in(and_6_out), .CLK(CLK), .clear(VC), .RES(RES), .value(V6));
  and and_7 (and_7_out, V6, and_6_out);
  COUNTER_BIT counter_bit_8 (.in(and_7_out), .CLK(CLK), .clear(VC), .RES(RES), .value(V7));
  and and_8 (and_8_out, V7, and_7_out);
  COUNTER_BIT counter_bit_9 (.in(and_8_out), .CLK(CLK), .clear(VC), .RES(RES), .value(V8));

  // Notes on the sheet:
  //   reduce propagation delay
endmodule

module HV_SELECT (
  input  H8,
  input  H7,
  input  H6,
  input  H5,
  input  H4,
  input  H3,
  input  H2,
  input  H1,
  input  H0,
  input  VB,
  input  BLNK,
  input  V8,
  input  V7,
  input  V6,
  input  V5,
  input  V4,
  input  V3,
  input  V2,
  input  V1,
  input  V0,
  output _279,
  output _256,
  output _65,
  output _0_7A,
  output _0_7B,
  output _335_339,
  output _63,
  output _255,
  output _0_63,
  output _256_319,
  output _0_255,
  output _0_1,
  output _6_7,
  output _4_5,
  output _336_340A,
  output _336_340B,
  output _2_3,
  output _270,
  output _328,
  output _279_2,
  output _304,
  output _323,
  output _308,
  output _340,
  output _247,
  output _244,
  output _261,
  output _241,
  output _241_2,
  output _0,
  output _240,
  output _261_2,
  output _261_3
);

  wire not_1_out, not_2_out, not_3_out, not_4_out, not_5_out, not_6_out, not_7_out, not_8_out, not_9_out,
       not_10_out, not_11_out, not_12_out, not_13_out, not_14_out, not_15_out, not_16_out, not_17_out,
       not_18_out;

  not not_1 (not_1_out, H8);
  not not_2 (not_2_out, H7);
  not not_3 (not_3_out, H6);
  not not_4 (not_4_out, H5);
  not not_5 (not_5_out, H4);
  not not_6 (not_6_out, H3);
  not not_7 (not_7_out, H2);
  not not_8 (not_8_out, H1);
  not not_9 (not_9_out, H0);
  not not_10 (not_10_out, V8);
  not not_11 (not_11_out, V7);
  not not_12 (not_12_out, V6);
  not not_13 (not_13_out, V5);
  not not_14 (not_14_out, V4);
  not not_15 (not_15_out, V3);
  not not_16 (not_16_out, V2);
  not not_17 (not_17_out, V1);
  not not_18 (not_18_out, V0);
  Pull_Resistor #(.pull(1)) pull_resistor_1 (.node(_279));
  Transistor #(.\type ("n")) transistor_1 (.in(1'b0), .out(_279), .gate(not_1_out));
  Transistor #(.\type ("n")) transistor_2 (.in(1'b0), .out(_279), .gate(H7));
  Transistor #(.\type ("n")) transistor_3 (.in(1'b0), .out(_279), .gate(H6));
  Transistor #(.\type ("n")) transistor_4 (.in(1'b0), .out(_279), .gate(H5));
  Transistor #(.\type ("n")) transistor_5 (.in(1'b0), .out(_279), .gate(not_5_out));
  Transistor #(.\type ("n")) transistor_6 (.in(1'b0), .out(_279), .gate(H3));
  Transistor #(.\type ("n")) transistor_7 (.in(1'b0), .out(_279), .gate(not_7_out));
  Transistor #(.\type ("n")) transistor_8 (.in(1'b0), .out(_279), .gate(not_8_out));
  Transistor #(.\type ("n")) transistor_9 (.in(1'b0), .out(_279), .gate(not_9_out));
  Pull_Resistor #(.pull(1)) pull_resistor_2 (.node(_247));
  Transistor #(.\type ("n")) transistor_10 (.in(1'b0), .out(_247), .gate(not_11_out));
  Transistor #(.\type ("n")) transistor_11 (.in(1'b0), .out(_247), .gate(not_12_out));
  Transistor #(.\type ("n")) transistor_12 (.in(1'b0), .out(_247), .gate(not_13_out));
  Transistor #(.\type ("n")) transistor_13 (.in(1'b0), .out(_247), .gate(not_14_out));
  Transistor #(.\type ("n")) transistor_14 (.in(1'b0), .out(_247), .gate(V3));
  Transistor #(.\type ("n")) transistor_15 (.in(1'b0), .out(_247), .gate(not_16_out));
  Transistor #(.\type ("n")) transistor_16 (.in(1'b0), .out(_247), .gate(not_17_out));
  Transistor #(.\type ("n")) transistor_17 (.in(1'b0), .out(_247), .gate(not_18_out));
  Pull_Resistor #(.pull(1)) pull_resistor_3 (.node(_256));
  Transistor #(.\type ("n")) transistor_18 (.in(1'b0), .out(_256), .gate(not_1_out));
  Transistor #(.\type ("n")) transistor_19 (.in(1'b0), .out(_256), .gate(H7));
  Transistor #(.\type ("n")) transistor_20 (.in(1'b0), .out(_256), .gate(H6));
  Transistor #(.\type ("n")) transistor_21 (.in(1'b0), .out(_256), .gate(H5));
  Transistor #(.\type ("n")) transistor_22 (.in(1'b0), .out(_256), .gate(H4));
  Transistor #(.\type ("n")) transistor_23 (.in(1'b0), .out(_256), .gate(H3));
  Transistor #(.\type ("n")) transistor_24 (.in(1'b0), .out(_256), .gate(H2));
  Transistor #(.\type ("n")) transistor_25 (.in(1'b0), .out(_256), .gate(H1));
  Transistor #(.\type ("n")) transistor_26 (.in(1'b0), .out(_256), .gate(H0));
  Pull_Resistor #(.pull(1)) pull_resistor_4 (.node(_244));
  Transistor #(.\type ("n")) transistor_27 (.in(1'b0), .out(_244), .gate(not_11_out));
  Transistor #(.\type ("n")) transistor_28 (.in(1'b0), .out(_244), .gate(not_12_out));
  Transistor #(.\type ("n")) transistor_29 (.in(1'b0), .out(_244), .gate(not_13_out));
  Transistor #(.\type ("n")) transistor_30 (.in(1'b0), .out(_244), .gate(not_14_out));
  Transistor #(.\type ("n")) transistor_31 (.in(1'b0), .out(_244), .gate(V3));
  Transistor #(.\type ("n")) transistor_32 (.in(1'b0), .out(_244), .gate(not_16_out));
  Transistor #(.\type ("n")) transistor_33 (.in(1'b0), .out(_244), .gate(V1));
  Transistor #(.\type ("n")) transistor_34 (.in(1'b0), .out(_244), .gate(V0));
  Pull_Resistor #(.pull(1)) pull_resistor_5 (.node(_65));
  Transistor #(.\type ("n")) transistor_35 (.in(1'b0), .out(_65), .gate(H8));
  Transistor #(.\type ("n")) transistor_36 (.in(1'b0), .out(_65), .gate(H7));
  Transistor #(.\type ("n")) transistor_37 (.in(1'b0), .out(_65), .gate(not_3_out));
  Transistor #(.\type ("n")) transistor_38 (.in(1'b0), .out(_65), .gate(H5));
  Transistor #(.\type ("n")) transistor_39 (.in(1'b0), .out(_65), .gate(H4));
  Transistor #(.\type ("n")) transistor_40 (.in(1'b0), .out(_65), .gate(H3));
  Transistor #(.\type ("n")) transistor_41 (.in(1'b0), .out(_65), .gate(H2));
  Transistor #(.\type ("n")) transistor_42 (.in(1'b0), .out(_65), .gate(H1));
  Transistor #(.\type ("n")) transistor_43 (.in(1'b0), .out(_65), .gate(not_9_out));
  Transistor #(.\type ("n")) transistor_44 (.in(1'b0), .out(_65), .gate(BLNK));
  Pull_Resistor #(.pull(1)) pull_resistor_6 (.node(_261));
  Transistor #(.\type ("n")) transistor_45 (.in(1'b0), .out(_261), .gate(not_10_out));
  Transistor #(.\type ("n")) transistor_46 (.in(1'b0), .out(_261), .gate(V7));
  Transistor #(.\type ("n")) transistor_47 (.in(1'b0), .out(_261), .gate(V6));
  Transistor #(.\type ("n")) transistor_48 (.in(1'b0), .out(_261), .gate(V5));
  Transistor #(.\type ("n")) transistor_49 (.in(1'b0), .out(_261), .gate(V4));
  Transistor #(.\type ("n")) transistor_50 (.in(1'b0), .out(_261), .gate(V3));
  Transistor #(.\type ("n")) transistor_51 (.in(1'b0), .out(_261), .gate(not_16_out));
  Transistor #(.\type ("n")) transistor_52 (.in(1'b0), .out(_261), .gate(V1));
  Transistor #(.\type ("n")) transistor_53 (.in(1'b0), .out(_261), .gate(not_18_out));
  Pull_Resistor #(.pull(1)) pull_resistor_7 (.node(_0_7A));
  Transistor #(.\type ("n")) transistor_54 (.in(1'b0), .out(_0_7A), .gate(H7));
  Transistor #(.\type ("n")) transistor_55 (.in(1'b0), .out(_0_7A), .gate(H6));
  Transistor #(.\type ("n")) transistor_56 (.in(1'b0), .out(_0_7A), .gate(H5));
  Transistor #(.\type ("n")) transistor_57 (.in(1'b0), .out(_0_7A), .gate(H4));
  Transistor #(.\type ("n")) transistor_58 (.in(1'b0), .out(_0_7A), .gate(H3));
  Pull_Resistor #(.pull(1)) pull_resistor_8 (.node(_241));
  Transistor #(.\type ("n")) transistor_59 (.in(1'b0), .out(_241), .gate(not_11_out));
  Transistor #(.\type ("n")) transistor_60 (.in(1'b0), .out(_241), .gate(not_12_out));
  Transistor #(.\type ("n")) transistor_61 (.in(1'b0), .out(_241), .gate(not_13_out));
  Transistor #(.\type ("n")) transistor_62 (.in(1'b0), .out(_241), .gate(not_14_out));
  Transistor #(.\type ("n")) transistor_63 (.in(1'b0), .out(_241), .gate(V3));
  Transistor #(.\type ("n")) transistor_64 (.in(1'b0), .out(_241), .gate(V2));
  Transistor #(.\type ("n")) transistor_65 (.in(1'b0), .out(_241), .gate(V1));
  Transistor #(.\type ("n")) transistor_66 (.in(1'b0), .out(_241), .gate(not_18_out));
  Pull_Resistor #(.pull(1)) pull_resistor_9 (.node(_335_339));
  Pull_Resistor #(.pull(1)) pull_resistor_10 (.node(_0_7B));
  Transistor #(.\type ("n")) transistor_67 (.in(1'b0), .out(_0_7B), .gate(H8));
  Transistor #(.\type ("n")) transistor_68 (.in(1'b0), .out(_335_339), .gate(not_1_out));
  Transistor #(.\type ("n")) transistor_69 (.in(1'b0), .out(_335_339), .gate(H7));
  Transistor #(.\type ("n")) transistor_70 (.in(1'b0), .out(_335_339), .gate(not_3_out));
  Transistor #(.\type ("n")) transistor_71 (.in(1'b0), .out(_335_339), .gate(H5));
  Transistor #(.\type ("n")) transistor_72 (.in(1'b0), .out(_335_339), .gate(not_5_out));
  Transistor #(.\type ("n")) transistor_73 (.in(1'b0), .out(_335_339), .gate(H3));
  Transistor #(.\type ("n")) transistor_74 (.in(1'b0), .out(_335_339), .gate(H2));
  Transistor #(.\type ("n")) transistor_75 (.in(1'b0), .out(_0_7B), .gate(VB));
  Pull_Resistor #(.pull(1)) pull_resistor_11 (.node(_0));
  Pull_Resistor #(.pull(1)) pull_resistor_12 (.node(_241_2));
  Transistor #(.\type ("n")) transistor_76 (.in(1'b0), .out(_0), .gate(V8));
  Transistor #(.\type ("n")) transistor_77 (.in(1'b0), .out(_0), .gate(V7));
  Transistor #(.\type ("n")) transistor_78 (.in(1'b0), .out(_241_2), .gate(not_11_out));
  Transistor #(.\type ("n")) transistor_79 (.in(1'b0), .out(_0), .gate(V6));
  Transistor #(.\type ("n")) transistor_80 (.in(1'b0), .out(_241_2), .gate(not_12_out));
  Transistor #(.\type ("n")) transistor_81 (.in(1'b0), .out(_0), .gate(V5));
  Transistor #(.\type ("n")) transistor_82 (.in(1'b0), .out(_241_2), .gate(not_13_out));
  Transistor #(.\type ("n")) transistor_83 (.in(1'b0), .out(_0), .gate(V4));
  Transistor #(.\type ("n")) transistor_84 (.in(1'b0), .out(_241_2), .gate(not_14_out));
  Transistor #(.\type ("n")) transistor_85 (.in(1'b0), .out(_0), .gate(V3));
  Transistor #(.\type ("n")) transistor_86 (.in(1'b0), .out(_241_2), .gate(V3));
  Transistor #(.\type ("n")) transistor_87 (.in(1'b0), .out(_241_2), .gate(V2));
  Transistor #(.\type ("n")) transistor_88 (.in(1'b0), .out(_0), .gate(V2));
  Transistor #(.\type ("n")) transistor_89 (.in(1'b0), .out(_0), .gate(V1));
  Transistor #(.\type ("n")) transistor_90 (.in(1'b0), .out(_241_2), .gate(V1));
  Transistor #(.\type ("n")) transistor_91 (.in(1'b0), .out(_0), .gate(V0));
  Transistor #(.\type ("n")) transistor_92 (.in(1'b0), .out(_241_2), .gate(not_18_out));
  Pull_Resistor #(.pull(1)) pull_resistor_13 (.node(_63));
  Transistor #(.\type ("n")) transistor_93 (.in(1'b0), .out(_63), .gate(H8));
  Transistor #(.\type ("n")) transistor_94 (.in(1'b0), .out(_63), .gate(H7));
  Transistor #(.\type ("n")) transistor_95 (.in(1'b0), .out(_63), .gate(H6));
  Transistor #(.\type ("n")) transistor_96 (.in(1'b0), .out(_63), .gate(not_4_out));
  Transistor #(.\type ("n")) transistor_97 (.in(1'b0), .out(_63), .gate(not_5_out));
  Transistor #(.\type ("n")) transistor_98 (.in(1'b0), .out(_63), .gate(not_6_out));
  Transistor #(.\type ("n")) transistor_99 (.in(1'b0), .out(_63), .gate(not_7_out));
  Transistor #(.\type ("n")) transistor_100 (.in(1'b0), .out(_63), .gate(not_8_out));
  Transistor #(.\type ("n")) transistor_101 (.in(1'b0), .out(_63), .gate(not_9_out));
  Pull_Resistor #(.pull(1)) pull_resistor_14 (.node(_240));
  Transistor #(.\type ("n")) transistor_102 (.in(1'b0), .out(_240), .gate(not_11_out));
  Transistor #(.\type ("n")) transistor_103 (.in(1'b0), .out(_240), .gate(not_12_out));
  Transistor #(.\type ("n")) transistor_104 (.in(1'b0), .out(_240), .gate(not_13_out));
  Transistor #(.\type ("n")) transistor_105 (.in(1'b0), .out(_240), .gate(not_14_out));
  Transistor #(.\type ("n")) transistor_106 (.in(1'b0), .out(_240), .gate(V3));
  Transistor #(.\type ("n")) transistor_107 (.in(1'b0), .out(_240), .gate(V2));
  Transistor #(.\type ("n")) transistor_108 (.in(1'b0), .out(_240), .gate(V1));
  Transistor #(.\type ("n")) transistor_109 (.in(1'b0), .out(_240), .gate(V0));
  Pull_Resistor #(.pull(1)) pull_resistor_15 (.node(_255));
  Transistor #(.\type ("n")) transistor_110 (.in(1'b0), .out(_255), .gate(not_2_out));
  Transistor #(.\type ("n")) transistor_111 (.in(1'b0), .out(_255), .gate(not_3_out));
  Transistor #(.\type ("n")) transistor_112 (.in(1'b0), .out(_255), .gate(not_4_out));
  Transistor #(.\type ("n")) transistor_113 (.in(1'b0), .out(_255), .gate(not_5_out));
  Transistor #(.\type ("n")) transistor_114 (.in(1'b0), .out(_255), .gate(not_6_out));
  Transistor #(.\type ("n")) transistor_115 (.in(1'b0), .out(_255), .gate(not_7_out));
  Transistor #(.\type ("n")) transistor_116 (.in(1'b0), .out(_255), .gate(not_8_out));
  Transistor #(.\type ("n")) transistor_117 (.in(1'b0), .out(_255), .gate(not_9_out));
  Pull_Resistor #(.pull(1)) pull_resistor_16 (.node(_261_2));
  Transistor #(.\type ("n")) transistor_118 (.in(1'b0), .out(_261_2), .gate(not_10_out));
  Transistor #(.\type ("n")) transistor_119 (.in(1'b0), .out(_261_2), .gate(V7));
  Transistor #(.\type ("n")) transistor_120 (.in(1'b0), .out(_261_2), .gate(V6));
  Transistor #(.\type ("n")) transistor_121 (.in(1'b0), .out(_261_2), .gate(V5));
  Transistor #(.\type ("n")) transistor_122 (.in(1'b0), .out(_261_2), .gate(V4));
  Transistor #(.\type ("n")) transistor_123 (.in(1'b0), .out(_261_2), .gate(V3));
  Transistor #(.\type ("n")) transistor_124 (.in(1'b0), .out(_261_2), .gate(not_16_out));
  Transistor #(.\type ("n")) transistor_125 (.in(1'b0), .out(_261_2), .gate(V1));
  Transistor #(.\type ("n")) transistor_126 (.in(1'b0), .out(_261_2), .gate(not_18_out));
  Pull_Resistor #(.pull(1)) pull_resistor_17 (.node(_0_63));
  Transistor #(.\type ("n")) transistor_127 (.in(1'b0), .out(_0_63), .gate(H8));
  Transistor #(.\type ("n")) transistor_128 (.in(1'b0), .out(_0_63), .gate(H7));
  Transistor #(.\type ("n")) transistor_129 (.in(1'b0), .out(_0_63), .gate(H6));
  Pull_Resistor #(.pull(1)) pull_resistor_18 (.node(_261_3));
  Transistor #(.\type ("n")) transistor_130 (.in(1'b0), .out(_261_3), .gate(not_10_out));
  Transistor #(.\type ("n")) transistor_131 (.in(1'b0), .out(_261_3), .gate(V7));
  Transistor #(.\type ("n")) transistor_132 (.in(1'b0), .out(_261_3), .gate(V6));
  Transistor #(.\type ("n")) transistor_133 (.in(1'b0), .out(_261_3), .gate(V5));
  Transistor #(.\type ("n")) transistor_134 (.in(1'b0), .out(_261_3), .gate(V4));
  Transistor #(.\type ("n")) transistor_135 (.in(1'b0), .out(_261_3), .gate(V3));
  Transistor #(.\type ("n")) transistor_136 (.in(1'b0), .out(_261_3), .gate(not_16_out));
  Transistor #(.\type ("n")) transistor_137 (.in(1'b0), .out(_261_3), .gate(V1));
  Transistor #(.\type ("n")) transistor_138 (.in(1'b0), .out(_261_3), .gate(not_18_out));
  Pull_Resistor #(.pull(1)) pull_resistor_19 (.node(_256_319));
  Transistor #(.\type ("n")) transistor_139 (.in(1'b0), .out(_256_319), .gate(not_1_out));
  Transistor #(.\type ("n")) transistor_140 (.in(1'b0), .out(_256_319), .gate(H7));
  Transistor #(.\type ("n")) transistor_141 (.in(1'b0), .out(_256_319), .gate(H6));
  Transistor #(.\type ("n")) transistor_142 (.in(1'b0), .out(_256_319), .gate(BLNK));
  Pull_Resistor #(.pull(1)) pull_resistor_20 (.node(_0_255));
  Transistor #(.\type ("n")) transistor_143 (.in(1'b0), .out(_0_255), .gate(H8));
  Transistor #(.\type ("n")) transistor_144 (.in(1'b0), .out(_0_255), .gate(VB));
  Transistor #(.\type ("n")) transistor_145 (.in(1'b0), .out(_0_255), .gate(BLNK));
  Pull_Resistor #(.pull(1)) pull_resistor_21 (.node(_0_1));
  Transistor #(.\type ("n")) transistor_146 (.in(1'b0), .out(_0_1), .gate(H2));
  Transistor #(.\type ("n")) transistor_147 (.in(1'b0), .out(_0_1), .gate(H1));
  Transistor #(.\type ("n")) transistor_148 (.in(1'b0), .out(_0_1), .gate(BLNK));
  Pull_Resistor #(.pull(1)) pull_resistor_22 (.node(_6_7));
  Pull_Resistor #(.pull(1)) pull_resistor_23 (.node(_4_5));
  Transistor #(.\type ("n")) transistor_149 (.in(1'b0), .out(_6_7), .gate(not_7_out));
  Transistor #(.\type ("n")) transistor_150 (.in(1'b0), .out(_4_5), .gate(not_7_out));
  Transistor #(.\type ("n")) transistor_151 (.in(1'b0), .out(_4_5), .gate(H1));
  Transistor #(.\type ("n")) transistor_152 (.in(1'b0), .out(_6_7), .gate(not_8_out));
  Pull_Resistor #(.pull(1)) pull_resistor_24 (.node(_336_340A));
  Transistor #(.\type ("n")) transistor_153 (.in(1'b0), .out(_336_340A), .gate(not_1_out));
  Transistor #(.\type ("n")) transistor_154 (.in(1'b0), .out(_336_340A), .gate(not_3_out));
  Transistor #(.\type ("n")) transistor_155 (.in(1'b0), .out(_336_340A), .gate(H5));
  Transistor #(.\type ("n")) transistor_156 (.in(1'b0), .out(_336_340A), .gate(H4));
  Transistor #(.\type ("n")) transistor_157 (.in(1'b0), .out(_336_340A), .gate(BLNK));
  Pull_Resistor #(.pull(1)) pull_resistor_25 (.node(_336_340B));
  Transistor #(.\type ("n")) transistor_158 (.in(1'b0), .out(_336_340B), .gate(H8));
  Transistor #(.\type ("n")) transistor_159 (.in(1'b0), .out(_336_340B), .gate(BLNK));
  Pull_Resistor #(.pull(1)) pull_resistor_26 (.node(_2_3));
  Transistor #(.\type ("n")) transistor_160 (.in(1'b0), .out(_2_3), .gate(H2));
  Transistor #(.\type ("n")) transistor_161 (.in(1'b0), .out(_2_3), .gate(not_8_out));
  Pull_Resistor #(.pull(1)) pull_resistor_27 (.node(_270));
  Transistor #(.\type ("n")) transistor_162 (.in(1'b0), .out(_270), .gate(not_1_out));
  Transistor #(.\type ("n")) transistor_163 (.in(1'b0), .out(_270), .gate(H7));
  Transistor #(.\type ("n")) transistor_164 (.in(1'b0), .out(_270), .gate(H6));
  Transistor #(.\type ("n")) transistor_165 (.in(1'b0), .out(_270), .gate(H5));
  Transistor #(.\type ("n")) transistor_166 (.in(1'b0), .out(_270), .gate(H4));
  Transistor #(.\type ("n")) transistor_167 (.in(1'b0), .out(_270), .gate(not_6_out));
  Transistor #(.\type ("n")) transistor_168 (.in(1'b0), .out(_270), .gate(not_7_out));
  Transistor #(.\type ("n")) transistor_169 (.in(1'b0), .out(_270), .gate(not_8_out));
  Transistor #(.\type ("n")) transistor_170 (.in(1'b0), .out(_270), .gate(H0));
  Pull_Resistor #(.pull(1)) pull_resistor_28 (.node(_328));
  Transistor #(.\type ("n")) transistor_171 (.in(1'b0), .out(_328), .gate(not_1_out));
  Transistor #(.\type ("n")) transistor_172 (.in(1'b0), .out(_328), .gate(H7));
  Transistor #(.\type ("n")) transistor_173 (.in(1'b0), .out(_328), .gate(not_3_out));
  Transistor #(.\type ("n")) transistor_174 (.in(1'b0), .out(_328), .gate(H5));
  Transistor #(.\type ("n")) transistor_175 (.in(1'b0), .out(_328), .gate(H4));
  Transistor #(.\type ("n")) transistor_176 (.in(1'b0), .out(_328), .gate(not_6_out));
  Transistor #(.\type ("n")) transistor_177 (.in(1'b0), .out(_328), .gate(H2));
  Transistor #(.\type ("n")) transistor_178 (.in(1'b0), .out(_328), .gate(H1));
  Transistor #(.\type ("n")) transistor_179 (.in(1'b0), .out(_328), .gate(H0));
  Pull_Resistor #(.pull(1)) pull_resistor_29 (.node(_279_2));
  Transistor #(.\type ("n")) transistor_180 (.in(1'b0), .out(_279_2), .gate(not_1_out));
  Transistor #(.\type ("n")) transistor_181 (.in(1'b0), .out(_279_2), .gate(H7));
  Transistor #(.\type ("n")) transistor_182 (.in(1'b0), .out(_279_2), .gate(H6));
  Transistor #(.\type ("n")) transistor_183 (.in(1'b0), .out(_279_2), .gate(H5));
  Transistor #(.\type ("n")) transistor_184 (.in(1'b0), .out(_279_2), .gate(not_5_out));
  Transistor #(.\type ("n")) transistor_185 (.in(1'b0), .out(_279_2), .gate(H3));
  Transistor #(.\type ("n")) transistor_186 (.in(1'b0), .out(_279_2), .gate(not_7_out));
  Transistor #(.\type ("n")) transistor_187 (.in(1'b0), .out(_279_2), .gate(not_8_out));
  Transistor #(.\type ("n")) transistor_188 (.in(1'b0), .out(_279_2), .gate(not_9_out));
  Pull_Resistor #(.pull(1)) pull_resistor_30 (.node(_323));
  Pull_Resistor #(.pull(1)) pull_resistor_31 (.node(_304));
  Transistor #(.\type ("n")) transistor_189 (.in(1'b0), .out(_323), .gate(not_1_out));
  Transistor #(.\type ("n")) transistor_190 (.in(1'b0), .out(_304), .gate(not_1_out));
  Transistor #(.\type ("n")) transistor_191 (.in(1'b0), .out(_323), .gate(H7));
  Transistor #(.\type ("n")) transistor_192 (.in(1'b0), .out(_304), .gate(H7));
  Transistor #(.\type ("n")) transistor_193 (.in(1'b0), .out(_304), .gate(H6));
  Transistor #(.\type ("n")) transistor_194 (.in(1'b0), .out(_323), .gate(not_3_out));
  Transistor #(.\type ("n")) transistor_195 (.in(1'b0), .out(_323), .gate(H5));
  Transistor #(.\type ("n")) transistor_196 (.in(1'b0), .out(_304), .gate(not_4_out));
  Transistor #(.\type ("n")) transistor_197 (.in(1'b0), .out(_323), .gate(H4));
  Transistor #(.\type ("n")) transistor_198 (.in(1'b0), .out(_304), .gate(not_5_out));
  Transistor #(.\type ("n")) transistor_199 (.in(1'b0), .out(_323), .gate(H3));
  Transistor #(.\type ("n")) transistor_200 (.in(1'b0), .out(_304), .gate(H3));
  Transistor #(.\type ("n")) transistor_201 (.in(1'b0), .out(_323), .gate(H2));
  Transistor #(.\type ("n")) transistor_202 (.in(1'b0), .out(_304), .gate(H2));
  Transistor #(.\type ("n")) transistor_203 (.in(1'b0), .out(_304), .gate(H1));
  Transistor #(.\type ("n")) transistor_204 (.in(1'b0), .out(_323), .gate(not_8_out));
  Transistor #(.\type ("n")) transistor_205 (.in(1'b0), .out(_304), .gate(H0));
  Transistor #(.\type ("n")) transistor_206 (.in(1'b0), .out(_323), .gate(not_9_out));
  Pull_Resistor #(.pull(1)) pull_resistor_32 (.node(_308));
  Transistor #(.\type ("n")) transistor_207 (.in(1'b0), .out(_308), .gate(not_1_out));
  Transistor #(.\type ("n")) transistor_208 (.in(1'b0), .out(_308), .gate(H7));
  Transistor #(.\type ("n")) transistor_209 (.in(1'b0), .out(_308), .gate(H6));
  Transistor #(.\type ("n")) transistor_210 (.in(1'b0), .out(_308), .gate(not_4_out));
  Transistor #(.\type ("n")) transistor_211 (.in(1'b0), .out(_308), .gate(not_5_out));
  Transistor #(.\type ("n")) transistor_212 (.in(1'b0), .out(_308), .gate(H3));
  Transistor #(.\type ("n")) transistor_213 (.in(1'b0), .out(_308), .gate(not_7_out));
  Transistor #(.\type ("n")) transistor_214 (.in(1'b0), .out(_308), .gate(H1));
  Transistor #(.\type ("n")) transistor_215 (.in(1'b0), .out(_308), .gate(H0));
  Pull_Resistor #(.pull(1)) pull_resistor_33 (.node(_340));
  Transistor #(.\type ("n")) transistor_216 (.in(1'b0), .out(_340), .gate(not_1_out));
  Transistor #(.\type ("n")) transistor_217 (.in(1'b0), .out(_340), .gate(H7));
  Transistor #(.\type ("n")) transistor_218 (.in(1'b0), .out(_340), .gate(not_3_out));
  Transistor #(.\type ("n")) transistor_219 (.in(1'b0), .out(_340), .gate(H5));
  Transistor #(.\type ("n")) transistor_220 (.in(1'b0), .out(_340), .gate(not_5_out));
  Transistor #(.\type ("n")) transistor_221 (.in(1'b0), .out(_340), .gate(H3));
  Transistor #(.\type ("n")) transistor_222 (.in(1'b0), .out(_340), .gate(not_7_out));
  Transistor #(.\type ("n")) transistor_223 (.in(1'b0), .out(_340), .gate(H1));
  Transistor #(.\type ("n")) transistor_224 (.in(1'b0), .out(_340), .gate(H0));
endmodule

module CONTROL_UNIT (
  input  PCLK,
  input  nOBCLIP,
  input  nBGCLIP,
  input  BLACK,
  input  _279,
  input  _256,
  input  _65,
  input  _0_7A,
  input  _0_7B,
  input  _336_339,
  input  _63,
  input  _255,
  input  _0_63,
  input  _256_319,
  input  _0_255,
  input  _0_1,
  input  _6_7,
  input  _4_5,
  input  _336_340A,
  input  _336_340B,
  input  _2_3,
  input  _270,
  input  _328,
  input  _279_2,
  input  _304,
  input  _323,
  input  _308,
  input  _247,
  input  _244,
  input  _261,
  input  _241,
  input  _241_2,
  input  _0,
  input  _240,
  input  _261_2,
  input  _261_3,
  input  RES,
  input  V8,
  input  _340,
  output S_EV,
  output CLIP_O,
  output CLIP_B,
  output _0_HPOS,
  output EVAL,
  output E_EV,
  output I_OAM2,
  output PAR_O,
  output nVIS,
  output F_NT,
  output F_TB,
  output F_TA,
  output nFO,
  output F_AT,
  output SC_CNT,
  output SYNC,
  output BURST,
  output PICTURE,
  output VSET,
  output VB,
  output BLNK,
  output VCLR,
  output VIN,
  output HC,
  output VC
);

  wire and_1_out, and_2_out, and_3_out, and_4_out, d_latch_1_not_q, d_latch_2_q, d_latch_3_not_q,
       d_latch_4_not_q, d_latch_4_q, d_latch_5_q, d_latch_6_not_q, d_latch_6_q, d_latch_7_not_q,
       d_latch_8_not_q, d_latch_9_not_q, d_latch_10_not_q, d_latch_11_not_q, d_latch_12_not_q, d_latch_13_q,
       d_latch_14_q, d_latch_15_not_q, d_latch_16_not_q, d_latch_17_not_q, d_latch_24_q, d_latch_25_q,
       d_latch_27_q, d_latch_28_q, d_latch_29_q, d_latch_32_not_q, d_latch_33_q, d_latch_34_q, d_latch_35_q,
       d_latch_36_q, d_latch_37_q, d_latch_38_q, d_latch_39_q, d_latch_40_not_q, multiplexer_1_out,
       multiplexer_2_out, nor_1_out, nor_2_out, nor_3_out, nor_4_out, nor_9_out, nor_13_out, nor_14_out,
       not_1_out, not_2_out, not_3_out, not_4_out, not_5_out, not_6_out, not_8_out, not_9_out, s_r_ff_1_q,
       s_r_ff_2_q, s_r_ff_3_q, s_r_ff_4_q, s_r_ff_5_q, s_r_ff_6_q, s_r_ff_7_q, s_r_ff_8_q;

  not not_1 (not_1_out, PCLK);
  D_latch d_latch_1 (.EN(not_1_out), .D(_65), .NOT_Q(d_latch_1_not_q));  // open: Q
  D_latch d_latch_2 (.EN(not_1_out), .D(_0_7A), .Q(d_latch_2_q));  // open: NOT_Q
  D_latch d_latch_3 (.EN(not_1_out), .D(_0_7B), .NOT_Q(d_latch_3_not_q));  // open: Q
  D_latch d_latch_4 (.EN(not_1_out), .D(_336_339), .Q(d_latch_4_q), .NOT_Q(d_latch_4_not_q));
  D_latch d_latch_5 (.EN(not_1_out), .D(_63), .Q(d_latch_5_q));  // open: NOT_Q
  D_latch d_latch_6 (.D(_255), .Q(d_latch_6_q), .NOT_Q(d_latch_6_not_q));  // open: EN
  D_latch d_latch_7 (.EN(not_1_out), .D(_0_63), .NOT_Q(d_latch_7_not_q));  // open: Q
  D_latch d_latch_8 (.EN(not_1_out), .D(_256_319), .NOT_Q(d_latch_8_not_q));  // open: Q
  D_latch d_latch_9 (.EN(not_1_out), .D(_0_255), .NOT_Q(d_latch_9_not_q));  // open: Q
  D_latch d_latch_10 (.EN(not_1_out), .D(_0_1), .NOT_Q(d_latch_10_not_q));  // open: Q
  D_latch d_latch_11 (.EN(not_1_out), .D(_6_7), .NOT_Q(d_latch_11_not_q));  // open: Q
  D_latch d_latch_12 (.EN(not_1_out), .D(_4_5), .NOT_Q(d_latch_12_not_q));  // open: Q
  D_latch d_latch_13 (.EN(not_1_out), .D(_336_340A), .Q(d_latch_13_q));  // open: NOT_Q
  D_latch d_latch_14 (.EN(not_1_out), .D(_336_340B), .Q(d_latch_14_q));  // open: NOT_Q
  D_latch d_latch_15 (.EN(not_1_out), .D(_2_3), .NOT_Q(d_latch_15_not_q));  // open: Q
  D_latch d_latch_16 (.EN(not_1_out), .D(_241_2), .NOT_Q(d_latch_16_not_q));  // open: Q
  D_latch d_latch_17 (.EN(not_1_out), .D(_261_3), .NOT_Q(d_latch_17_not_q));  // open: Q
  S_R_Flip_Flop #(.trigger("high")) s_r_ff_1 (
    .S(_279), .clk(not_1_out), .R(_256), .Q(s_r_ff_1_q));  // open: Qn, preset, reset, en
  D_latch d_latch_18 (.EN(PCLK), .D(d_latch_1_not_q), .NOT_Q(S_EV));  // open: Q
  nor nor_1 (nor_1_out, d_latch_2_q, d_latch_3_not_q);
  D_latch d_latch_19 (.EN(PCLK), .D(d_latch_4_not_q), .NOT_Q(_0_HPOS));  // open: Q
  nor nor_2 (nor_2_out, d_latch_4_q, d_latch_5_q, d_latch_6_q);
  D_latch d_latch_20 (.EN(PCLK), .D(d_latch_7_not_q), .NOT_Q(I_OAM2));  // open: Q
  D_latch d_latch_21 (.EN(PCLK), .D(d_latch_8_not_q), .NOT_Q(PAR_O));  // open: Q
  D_latch d_latch_22 (.EN(PCLK), .D(d_latch_9_not_q), .Q(nVIS));  // open: NOT_Q
  D_latch d_latch_23 (.EN(PCLK), .D(d_latch_10_not_q), .Q(F_NT));  // open: NOT_Q
  D_latch d_latch_24 (.EN(PCLK), .D(d_latch_11_not_q), .Q(d_latch_24_q));  // open: NOT_Q
  D_latch d_latch_25 (.EN(PCLK), .D(d_latch_12_not_q), .Q(d_latch_25_q));  // open: NOT_Q
  nor nor_3 (nor_3_out, d_latch_13_q, d_latch_14_q);
  S_R_Flip_Flop #(.trigger("high")) s_r_ff_2 (
    .S(_270), .clk(not_1_out), .R(_328), .Q(s_r_ff_2_q));  // open: Qn, preset, reset, en
  S_R_Flip_Flop #(.trigger("high")) s_r_ff_3 (
    .S(_279_2), .clk(not_1_out), .R(_304), .Q(s_r_ff_3_q));  // open: Qn, preset, reset, en
  S_R_Flip_Flop #(.trigger("high")) s_r_ff_4 (
    .S(_323), .clk(not_1_out), .R(_308), .Q(s_r_ff_4_q));  // open: Qn, preset, reset, en
  S_R_Flip_Flop #(.trigger("high")) s_r_ff_5 (
    .S(_0), .clk(not_1_out), .R(_240), .Q(s_r_ff_5_q));  // open: Qn, preset, reset, en
  S_R_Flip_Flop #(.trigger("high")) s_r_ff_6 (
    .S(_240), .clk(not_1_out), .R(_261_2), .Q(s_r_ff_6_q));  // open: Qn, preset, reset, en
  D_latch d_latch_26 (.EN(PCLK), .D(d_latch_17_not_q), .NOT_Q(VCLR));  // open: Q
  nor nor_4 (nor_4_out, not_6_out, RES);
  D_latch d_latch_27 (.EN(PCLK), .D(nor_3_out), .Q(d_latch_27_q), .NOT_Q(nFO));
  nor nor_5 (F_AT, nor_3_out, d_latch_15_not_q);
  and and_1 (and_1_out, s_r_ff_3_q, _247);
  and and_2 (and_2_out, s_r_ff_3_q, _244);
  and and_3 (and_3_out, s_r_ff_2_q, _261);
  and and_4 (and_4_out, s_r_ff_2_q, _241);
  not not_2 (not_2_out, VCLR);
  Multiplexer multiplexer_1 (.in0(nor_4_out), .in1(not_8_out), .out(multiplexer_1_out), .sel(V8));  // open: en
  D_latch d_latch_28 (.EN(PCLK), .D(nor_1_out), .Q(d_latch_28_q));  // open: NOT_Q
  D_latch d_latch_29 (.EN(PCLK), .D(nor_1_out), .Q(d_latch_29_q));  // open: NOT_Q
  D_latch d_latch_30 (.EN(PCLK), .D(nor_2_out), .Q(EVAL));  // open: NOT_Q
  D_latch d_latch_31 (.EN(PCLK), .D(d_latch_6_not_q), .NOT_Q(E_EV));  // open: Q
  not not_3 (not_3_out, s_r_ff_3_q);
  not not_4 (not_4_out, s_r_ff_1_q);
  S_R_Flip_Flop #(.trigger("high")) s_r_ff_7 (
    .S(and_2_out), .clk(1'b1), .R(and_1_out), .Q(s_r_ff_7_q));  // open: Qn, preset, reset, en
  S_R_Flip_Flop #(.trigger("high")) s_r_ff_8 (
    .S(and_4_out), .clk(1'b1), .R(and_3_out), .Q(s_r_ff_8_q));  // open: Qn, preset, reset, en
  D_latch d_latch_32 (.EN(PCLK), .D(d_latch_16_not_q), .NOT_Q(d_latch_32_not_q));  // open: Q
  not not_5 (not_5_out, _336_339);
  not not_6 (not_6_out, multiplexer_1_out);
  nor nor_6 (F_TB, d_latch_24_q, d_latch_27_q);
  nor nor_7 (F_TA, d_latch_25_q, d_latch_27_q);
  nor nor_8 (SC_CNT, BLACK, not_3_out);
  D_latch d_latch_33 (.EN(PCLK), .D(not_4_out), .Q(d_latch_33_q));  // open: NOT_Q
  D_latch d_latch_34 (.EN(PCLK), .D(s_r_ff_4_q), .Q(d_latch_34_q));  // open: NOT_Q
  D_latch d_latch_35 (.EN(not_1_out), .D(d_latch_32_not_q), .Q(d_latch_35_q));  // open: NOT_Q
  not not_7 (VB, s_r_ff_5_q);
  or or_1 (BLNK, BLACK, s_r_ff_6_q);
  nor nor_9 (nor_9_out, not_5_out, not_2_out, nor_4_out);
  nor nor_10 (CLIP_O, d_latch_28_q, nOBCLIP);
  nor nor_11 (CLIP_B, d_latch_29_q, nBGCLIP);
  nor nor_12 (SYNC, d_latch_38_q, d_latch_33_q);
  nor nor_13 (nor_13_out, s_r_ff_3_q, s_r_ff_7_q);
  D_latch d_latch_36 (.EN(PCLK), .D(s_r_ff_2_q), .Q(d_latch_36_q));  // open: NOT_Q
  D_latch d_latch_37 (.EN(PCLK), .D(s_r_ff_8_q), .Q(d_latch_37_q));  // open: NOT_Q
  nor nor_14 (nor_14_out, _340, nor_9_out);
  not not_8 (not_8_out, not_9_out);
  Multiplexer multiplexer_2 (.in0(not_6_out), .in1(not_8_out), .out(multiplexer_2_out), .sel(V8));  // open: en
  not not_9 (not_9_out, multiplexer_2_out);
  nor nor_15 (BURST, SYNC, d_latch_34_q);
  D_latch d_latch_38 (.EN(PCLK), .D(nor_13_out), .Q(d_latch_38_q));  // open: NOT_Q
  or or_2 (PICTURE, d_latch_36_q, d_latch_37_q);
  nor nor_16 (VSET, not_1_out, d_latch_35_q, d_latch_16_not_q);
  D_latch d_latch_39 (.EN(not_1_out), .D(nor_14_out), .Q(d_latch_39_q), .NOT_Q(HC));
  D_latch d_latch_40 (.EN(not_1_out), .D(_261), .NOT_Q(d_latch_40_not_q));  // open: Q
  nor nor_17 (VC, d_latch_39_q, d_latch_40_not_q);

  assign VIN = _340;

  // Notes on the sheet:
  //   HPOS control
  //   VPOS control
  //   H/V control
  //   Front porch RS flip/flop
  //   /HB
  //   BPORCH
  //   Back porch flip/flop
  //   /HB
  //   /VSET
  //   BLACK
  //   BLACK
  //   ODD/EVEN flip/flop
  //   BPORCH
  //   VSYNC
  //   /FPORCH
  //   /FPORCH
endmodule

module REGISTER_SELECT (
  input  nDBE,
  input  RC,
  input  RS0,
  input  RS1,
  input  RS2,
  input  R_W,
  output nW6_1,
  output nW6_2,
  output nW5_1,
  output nW5_2,
  output nR7,
  output nW7,
  output nW4,
  output nW3,
  output nR2,
  output nW1,
  output nW0,
  output nR4
);

  wire multiplexer_1_out, multiplexer_2_out, nor_1_out, nor_2_out, nor_3_out, nor_4_out, nor_5_out,
       nor_6_out, nor_7_out, nor_8_out, nor_9_out, nor_10_out, nor_11_out, nor_12_out, nor_13_out,
       nor_14_out, nor_15_out, nor_16_out, nor_17_out, not_1_out, not_2_out, not_3_out, not_4_out, not_5_out,
       not_6_out;

  not not_1 (not_1_out, RS0);
  not not_2 (not_2_out, RS1);
  not not_3 (not_3_out, RS2);
  not not_4 (not_4_out, R_W);
  nor nor_1 (nor_1_out, nor_16_out, RC, multiplexer_1_out);
  Multiplexer multiplexer_1 (.in0(not_6_out), .in1(not_5_out), .out(multiplexer_1_out), .sel(nor_15_out));  // open: en
  not not_5 (not_5_out, nor_1_out);
  Multiplexer multiplexer_2 (.in0(not_6_out), .in1(nor_1_out), .out(multiplexer_2_out), .sel(nor_15_out));  // open: en
  nor nor_2 (nor_2_out, multiplexer_2_out, RC, nor_16_out);
  not not_6 (not_6_out, nor_2_out);
  nor nor_3 (nor_3_out, RS0, not_2_out, not_3_out, R_W, nor_1_out);
  nor nor_4 (nor_4_out, RS0, not_2_out, not_3_out, R_W, not_5_out);
  nor nor_5 (nor_5_out, not_1_out, RS1, not_3_out, R_W, nor_1_out);
  nor nor_6 (nor_6_out, not_1_out, RS1, not_3_out, R_W, not_5_out);
  not not_7 (nR7, nor_7_out);
  nor nor_7 (nor_7_out, not_1_out, not_2_out, not_3_out, not_4_out);
  not not_8 (nW7, nor_8_out);
  nor nor_8 (nor_8_out, not_1_out, not_2_out, not_3_out, R_W);
  nor nor_9 (nor_9_out, RS0, RS1, not_3_out, R_W);
  not not_9 (nW4, nor_9_out);
  nor nor_10 (nor_10_out, not_1_out, not_2_out, RS2, R_W);
  not not_10 (nW3, nor_10_out);
  nor nor_11 (nor_11_out, RS0, not_2_out, RS2, not_4_out);
  not not_11 (nR2, nor_11_out);
  nor nor_12 (nor_12_out, not_1_out, RS1, RS2, R_W);
  not not_12 (nW1, nor_12_out);
  nor nor_13 (nor_13_out, RS0, RS1, RS2, R_W);
  not not_13 (nW0, nor_13_out);
  nor nor_14 (nor_14_out, RS0, RS1, not_3_out, not_4_out);
  not not_14 (nR4, nor_14_out);
  nor nor_15 (nor_15_out, nDBE, nor_17_out);
  nor nor_16 (nor_16_out, nDBE, nR2);
  not not_15 (nW6_1, nor_3_out);
  not not_16 (nW6_2, nor_4_out);
  not not_17 (nW5_1, nor_5_out);
  not not_18 (nW5_2, nor_6_out);
  nor nor_17 (nor_17_out, nor_3_out, nor_4_out, nor_5_out, nor_6_out);

  // Notes on the sheet:
  //   1ST
  //   2ND
  //   $2005/$2006 first/second write latch
  //   W5/6
  //   R2
endmodule

module VIDEO_OUT (
  input  CLK,
  input  RES,
  input  nTR,
  input  nTG,
  input  nTB,
  input  PCLK,
  input  nCC0,
  input  nCC1,
  input  nCC2,
  input  nCC3,
  input  SYNC,
  input  BURST,
  input  PICTURE,
  input  nLL0,
  input  nLL1,
  output [10:0] out_16
);

  wire d_latch_1_not_q, d_latch_2_not_q, d_latch_3_not_q, d_latch_4_not_q, d_latch_5_not_q, d_latch_6_not_q,
       d_latch_7_not_q, d_latch_8_q, d_latch_9_q, d_latch_10_not_q, d_latch_11_not_q, d_latch_12_not_q,
       d_latch_13_not_q, d_latch_14_q, d_latch_15_q, d_latch_16_q, d_latch_17_not_q, d_latch_18_q,
       d_latch_19_not_q, d_latch_20_q, d_latch_21_not_q, d_latch_22_q, d_latch_23_not_q, d_latch_24_q,
       d_latch_25_not_q, nor_1_out, nor_2_out, nor_3_out, nor_4_out, nor_5_out, nor_6_out, nor_7_out,
       nor_8_out, nor_9_out, nor_10_out, nor_11_out, nor_12_out, nor_13_out, nor_14_out, nor_15_out,
       nor_16_out, nor_17_out, nor_18_out, nor_19_out, nor_20_out, nor_21_out, nor_22_out, nor_23_out,
       nor_24_out, nor_25_out, nor_26_out, nor_27_out, nor_28_out, nor_29_out, nor_30_out, nor_31_out,
       nor_32_out, nor_33_out, nor_34_out, nor_35_out, nor_36_out, nor_37_out, nor_38_out, nor_39_out,
       nor_40_out, nor_41_out, nor_42_out, nor_43_out, not_1_out, not_2_out, not_3_out, not_4_out, not_5_out,
       not_6_out, not_7_out, not_8_out, not_9_out, not_10_out, not_11_out, not_12_out, not_13_out,
       not_15_out, not_17_out, not_18_out, not_26_out, or_1_out;

  not not_1 (not_1_out, PCLK);
  D_latch d_latch_1 (.EN(PCLK), .D(nCC0), .NOT_Q(d_latch_1_not_q));  // open: Q
  D_latch d_latch_2 (.EN(PCLK), .D(nCC1), .NOT_Q(d_latch_2_not_q));  // open: Q
  D_latch d_latch_3 (.EN(PCLK), .D(nCC2), .NOT_Q(d_latch_3_not_q));  // open: Q
  D_latch d_latch_4 (.EN(PCLK), .D(nCC3), .NOT_Q(d_latch_4_not_q));  // open: Q
  nor nor_1 (nor_1_out, nor_7_out, PICTURE);
  not not_2 (not_2_out, nLL0);
  not not_3 (not_3_out, nLL1);
  nor nor_2 (nor_2_out, d_latch_10_not_q, nTR, nor_11_out);
  nor nor_3 (nor_3_out, d_latch_10_not_q, nTG, nor_34_out);
  nor nor_4 (nor_4_out, d_latch_10_not_q, nTB, nor_24_out);
  D_latch d_latch_5 (.EN(not_1_out), .D(d_latch_1_not_q), .NOT_Q(d_latch_5_not_q));  // open: Q
  D_latch d_latch_6 (.EN(not_1_out), .D(d_latch_2_not_q), .NOT_Q(d_latch_6_not_q));  // open: Q
  D_latch d_latch_7 (.EN(not_1_out), .D(d_latch_3_not_q), .NOT_Q(d_latch_7_not_q));  // open: Q
  D_latch d_latch_8 (.EN(not_1_out), .D(d_latch_4_not_q), .Q(d_latch_8_q));  // open: NOT_Q
  D_latch d_latch_9 (.EN(not_1_out), .D(or_1_out), .Q(d_latch_9_q));  // open: NOT_Q
  or or_1 (or_1_out, SYNC, BURST, nor_1_out);
  not not_4 (not_4_out, SYNC);
  nor nor_5 (nor_5_out, nor_2_out, nor_3_out, nor_4_out);
  not not_5 (not_5_out, nor_5_out);
  nor nor_6 (nor_6_out, d_latch_8_q, d_latch_9_q);
  D_latch d_latch_10 (.EN(not_1_out), .D(nor_1_out), .NOT_Q(d_latch_10_not_q));  // open: Q
  D_latch d_latch_11 (.EN(not_1_out), .D(not_4_out), .NOT_Q(d_latch_11_not_q));  // open: Q
  D_latch d_latch_12 (.EN(not_1_out), .D(BURST), .NOT_Q(d_latch_12_not_q));  // open: Q
  nor nor_7 (nor_7_out, d_latch_6_not_q, d_latch_7_not_q, nor_6_out);
  not not_6 (not_6_out, d_latch_19_not_q);
  not not_7 (not_7_out, d_latch_5_not_q);
  not not_8 (not_8_out, d_latch_6_not_q);
  not not_9 (not_9_out, d_latch_7_not_q);
  not not_10 (not_10_out, nor_6_out);
  D_latch d_latch_13 (.EN(not_1_out), .D(or_1_out), .NOT_Q(d_latch_13_not_q));  // open: Q
  not not_11 (not_11_out, nor_8_out);
  nor nor_8 (nor_8_out, d_latch_10_not_q, not_2_out, not_3_out);
  not not_12 (not_12_out, CLK);
  not not_13 (not_13_out, nor_9_out);
  nor nor_9 (nor_9_out, d_latch_10_not_q, nLL0, nLL1);
  D_latch d_latch_14 (.EN(not_12_out), .D(not_6_out), .Q(d_latch_14_q));  // open: NOT_Q
  nor nor_10 (nor_10_out, not_6_out, d_latch_17_not_q);
  not not_14 (out_16[0], not_5_out);
  not not_15 (not_15_out, d_latch_13_not_q);
  not not_16 (out_16[10], d_latch_11_not_q);
  nor nor_11 (nor_11_out, d_latch_14_q, RES);
  nor nor_12 (nor_12_out, nor_11_out, not_7_out, not_8_out, d_latch_7_not_q, nor_6_out);
  not not_17 (not_17_out, nor_13_out);
  nor nor_13 (nor_13_out, d_latch_10_not_q, not_2_out, nLL1);
  D_latch d_latch_15 (.EN(CLK), .D(nor_11_out), .Q(d_latch_15_q));  // open: NOT_Q
  not not_18 (not_18_out, nor_14_out);
  nor nor_14 (nor_14_out, d_latch_10_not_q, nLL0, not_3_out);
  nor nor_15 (nor_15_out, d_latch_15_q, nor_10_out);
  nor nor_16 (nor_16_out, nor_15_out, d_latch_5_not_q, not_8_out, d_latch_7_not_q, not_10_out);
  D_latch d_latch_16 (.EN(not_12_out), .D(nor_15_out), .Q(d_latch_16_q));  // open: NOT_Q
  nor nor_17 (nor_17_out, nor_43_out, d_latch_12_not_q);
  nor nor_18 (nor_18_out, d_latch_12_not_q, nor_17_out);
  nor nor_19 (nor_19_out, d_latch_16_q, RES);
  nor nor_20 (nor_20_out, nor_19_out, not_7_out, d_latch_6_not_q, not_9_out, nor_6_out);
  not not_19 (out_16[6], nor_17_out);
  not not_20 (out_16[9], nor_18_out);
  D_latch d_latch_17 (.EN(CLK), .D(nor_19_out), .NOT_Q(d_latch_17_not_q));  // open: Q
  nor nor_21 (nor_21_out, d_latch_17_not_q, d_latch_5_not_q, d_latch_6_not_q, not_9_out, not_10_out);
  or or_2 (out_16[7], not_15_out, not_26_out);
  D_latch d_latch_18 (.EN(not_12_out), .D(d_latch_17_not_q), .Q(d_latch_18_q));  // open: NOT_Q
  nor nor_22 (nor_22_out, nor_43_out, not_11_out);
  nor nor_23 (nor_23_out, not_11_out, nor_22_out);
  nor nor_24 (nor_24_out, d_latch_18_q, RES);
  nor nor_25 (nor_25_out, nor_24_out, not_7_out, not_8_out, not_9_out, nor_6_out);
  not not_21 (out_16[4], nor_22_out);
  not not_22 (out_16[8], nor_23_out);
  D_latch d_latch_19 (.EN(CLK), .D(nor_24_out), .NOT_Q(d_latch_19_not_q));  // open: Q
  D_latch d_latch_20 (.EN(not_12_out), .D(d_latch_19_not_q), .Q(d_latch_20_q));  // open: NOT_Q
  nor nor_26 (nor_26_out, d_latch_19_not_q, d_latch_5_not_q, not_8_out, not_9_out, not_10_out);
  nor nor_27 (nor_27_out, nor_43_out, not_13_out);
  nor nor_28 (nor_28_out, not_13_out, nor_27_out);
  nor nor_29 (nor_29_out, d_latch_20_q, RES);
  not not_23 (out_16[1], nor_27_out);
  not not_24 (out_16[2], nor_28_out);
  D_latch d_latch_21 (.EN(CLK), .D(nor_29_out), .NOT_Q(d_latch_21_not_q));  // open: Q
  nor nor_30 (nor_30_out, nor_29_out, not_7_out, d_latch_6_not_q, d_latch_7_not_q, not_10_out);
  D_latch d_latch_22 (.EN(not_12_out), .D(d_latch_21_not_q), .Q(d_latch_22_q));  // open: NOT_Q
  nor nor_31 (nor_31_out, d_latch_21_not_q, d_latch_5_not_q, d_latch_6_not_q, not_9_out, nor_6_out);
  nor nor_32 (nor_32_out, nor_43_out, not_18_out);
  nor nor_33 (nor_33_out, not_18_out, nor_32_out);
  nor nor_34 (nor_34_out, d_latch_22_q, RES);
  D_latch d_latch_23 (.EN(CLK), .D(nor_34_out), .NOT_Q(d_latch_23_not_q));  // open: Q
  not not_25 (out_16[3], nor_32_out);
  not not_26 (not_26_out, nor_33_out);
  D_latch d_latch_24 (.EN(not_12_out), .D(d_latch_23_not_q), .Q(d_latch_24_q));  // open: NOT_Q
  nor nor_35 (nor_35_out, nor_34_out, not_7_out, not_8_out, d_latch_7_not_q, not_10_out);
  nor nor_36 (nor_36_out, d_latch_24_q, RES);
  nor nor_37 (nor_37_out, nor_43_out, not_17_out);
  not not_27 (out_16[1], nor_37_out);
  nor nor_38 (nor_38_out, not_17_out, nor_37_out);
  not not_28 (out_16[5], nor_38_out);
  D_latch d_latch_25 (.EN(CLK), .D(nor_36_out), .NOT_Q(d_latch_25_not_q));  // open: Q
  nor nor_39 (nor_39_out, d_latch_23_not_q, d_latch_5_not_q, not_8_out, not_9_out, nor_6_out);
  nor nor_40 (nor_40_out, nor_36_out, not_7_out, d_latch_6_not_q, not_9_out, not_10_out);
  nor nor_41 (nor_41_out, d_latch_25_not_q, d_latch_5_not_q, d_latch_6_not_q, d_latch_7_not_q, not_10_out);
  nor nor_42 (nor_42_out, not_7_out, not_8_out, not_9_out, not_10_out);
  nor nor_43 (nor_43_out, nor_41_out, nor_40_out, nor_39_out, nor_35_out, nor_31_out, nor_30_out, nor_42_out, nor_26_out, nor_25_out, nor_21_out, nor_20_out, nor_16_out, nor_12_out);

  // Notes on the sheet:
  //   Emphasis
  //   TINT
  //   /POUT
  //   /POUT
  //   0
  //   1
  //   2
  //   3
  //   /PR
  //   /PB
  //   /PG
  //   /LU3
  //   P123
  //   TINT
  //   Color 1D (black)
  //   Synch
  //   Color burst
  //   /LU0
  //   /LU1
  //   /LU2
  //   /PZ
  //   /PZ
endmodule

module RW_CONTROL (
  input  R_W,
  input  nDBE,
  output nRD,
  output nWR
);

  wire nor_1_out, nor_2_out, not_1_out;

  not not_1 (not_1_out, R_W);
  nor nor_1 (nor_1_out, not_1_out, nDBE);
  not not_2 (nRD, nor_1_out);
  not not_3 (nWR, nor_2_out);
  nor nor_2 (nor_2_out, R_W, nDBE);

  // Notes on the sheet:
  //   R/W = 0: write data to PPU
  //   /RD = 0: CPU read data from PPU
  //   /WR = 0: CPU write data to PPU
endmodule

module CPU_DATA_PAD (
  input  nRD,
  input  nWR,
  input  PPU_CPU,
  input  PPU_data_in,
  output PPU_data_out,
  output CPU_PPU
);

  wire not_1_out, not_2_out;

  not not_1 (not_1_out, nRD);
  not not_2 (not_2_out, nWR);
  assign PPU_data_out = not_1_out ? PPU_CPU : 1'bz;  // Controlled_Buffer controlled_buffer_1
  assign CPU_PPU = not_2_out ? PPU_data_in : 1'bz;  // Controlled_Buffer controlled_buffer_2

  // Notes on the sheet:
  //   /RD = 0: CPU read data from PPU
  //   /WR = 0: CPU write data to PPU
endmodule

module INTERRUPT_CONTROL (
  input  VSET,
  input  VCLR,
  input  nDBE,
  input  nR2,
  input  VBL_EN,
  output INT,
  output DB7
);

  wire d_latch_1_q, nor_1_out, not_1_out, or_1_out, s_r_ff_1_q;

  nor nor_1 (nor_1_out, nDBE, nR2);
  or or_1 (or_1_out, VCLR, nor_1_out);
  S_R_Flip_Flop #(.trigger("high")) s_r_ff_1 (
    .S(VSET), .clk(1'b1), .R(or_1_out), .Q(s_r_ff_1_q));  // open: Qn, preset, reset, en
  not not_1 (not_1_out, nor_1_out);
  and and_1 (INT, s_r_ff_1_q, VBL_EN);
  D_latch d_latch_1 (.EN(not_1_out), .D(s_r_ff_1_q), .Q(d_latch_1_q));  // open: NOT_Q
  assign DB7 = nor_1_out ? d_latch_1_q : 1'bz;  // Controlled_Buffer controlled_buffer_1

  // Notes on the sheet:
  //   R2_EN
  //   VBLANK FLIP/FLOP
endmodule

module COLOR_BUFFER_BIT (
  input  PCLK,
  input  CB_DB,
  input  RAM_CB,
  input  OE,
  input  DB_CB,
  input  DB,
  output DB_2,
  output nout,
  output CB_RAM
);

  wire and_1_out, d_latch_1_q, d_latch_2_not_q, d_latch_3_not_q, nand_1_out, nor_1_out, nor_2_out, not_1_out,
       not_2_out;

  not not_1 (not_1_out, PCLK);
  D_latch d_latch_1 (.EN(PCLK), .D(1'b1), .Q(d_latch_1_q));  // open: NOT_Q
  not not_2 (not_2_out, PCLK);
  D_latch d_latch_2 (.EN(not_1_out), .D(nout), .NOT_Q(d_latch_2_not_q));  // open: Q
  and and_1 (and_1_out, not_2_out, nor_2_out);
  D_latch d_latch_3 (.EN(PCLK), .D(d_latch_2_not_q), .NOT_Q(d_latch_3_not_q));  // open: Q
  nor nor_1 (nor_1_out, d_latch_1_q, and_1_out);
  nor nor_2 (nor_2_out, nor_1_out, RAM_CB);
  assign CB_RAM = DB_CB ? DB : 1'bz;  // Controlled_Buffer controlled_buffer_1
  assign DB_2 = CB_DB ? d_latch_3_not_q : 1'bz;  // Controlled_Buffer controlled_buffer_2
  nand nand_1 (nand_1_out, nor_2_out, OE);
  not not_3 (nout, nand_1_out);
endmodule
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module BG_COLOR (
  input  PCLK,
  input  PD0,
  input  PD1,
  input  PD2,
  input  PD3,
  input  PD4,
  input  PD5,
  input  PD6,
  input  PD7,
  input  CLPB,
  input  F_TA,
  input  F_TB,
  input  F_AT,
  input  nFO,
  input  H0,
  input  TVO1,
  input  THO1,
  input  FH0,
  input  FH1,
  input  FH2,
  output BGC0,
  output BGC1,
  output BGC2,
  output BGC3
);

  wire controlled_buffer_1_out, controlled_buffer_2_out, controlled_buffer_3_out, controlled_buffer_4_out,
       controlled_buffer_5_out, controlled_buffer_7_out, controlled_buffer_8_out, controlled_buffer_9_out,
       controlled_buffer_10_out, controlled_buffer_12_out, controlled_buffer_13_out,
       controlled_buffer_16_out, controlled_buffer_18_out, controlled_buffer_19_out,
       controlled_buffer_21_out, controlled_buffer_22_out, controlled_buffer_23_out,
       controlled_buffer_24_out, controlled_buffer_26_out, controlled_buffer_28_out,
       controlled_buffer_29_out, controlled_buffer_31_out, controlled_buffer_33_out,
       controlled_buffer_34_out, controlled_buffer_36_out, controlled_buffer_38_out,
       controlled_buffer_39_out, controlled_buffer_41_out, controlled_buffer_43_out,
       controlled_buffer_45_out, controlled_buffer_46_out, controlled_buffer_47_out,
       controlled_buffer_48_out, controlled_buffer_49_out, controlled_buffer_51_out,
       controlled_buffer_53_out, controlled_buffer_54_out, controlled_buffer_56_out,
       controlled_buffer_58_out, controlled_buffer_59_out, controlled_buffer_61_out,
       controlled_buffer_62_out, controlled_buffer_64_out, controlled_buffer_66_out,
       controlled_buffer_67_out, controlled_buffer_69_out, controlled_buffer_70_out,
       controlled_buffer_72_out, controlled_buffer_74_out, controlled_buffer_75_out,
       controlled_buffer_77_out, controlled_buffer_79_out, controlled_buffer_80_out,
       controlled_buffer_81_out, controlled_buffer_82_out, controlled_buffer_84_out,
       controlled_buffer_85_out, controlled_buffer_87_out, controlled_buffer_88_out,
       controlled_buffer_90_out, controlled_buffer_92_out, controlled_buffer_93_out,
       controlled_buffer_95_out, controlled_buffer_96_out, controlled_buffer_98_out,
       controlled_buffer_100_out, controlled_buffer_101_out, controlled_buffer_103_out,
       controlled_buffer_104_out, controlled_buffer_105_out, controlled_buffer_108_out,
       controlled_buffer_109_out, controlled_buffer_111_out, controlled_buffer_113_out,
       controlled_buffer_114_out, controlled_buffer_115_out, controlled_buffer_116_out,
       controlled_buffer_118_out, controlled_buffer_119_out, controlled_buffer_121_out,
       controlled_buffer_123_out, controlled_buffer_124_out, controlled_buffer_126_out,
       controlled_buffer_127_out, controlled_buffer_129_out, controlled_buffer_131_out,
       controlled_buffer_132_out, controlled_buffer_134_out, controlled_buffer_135_out,
       controlled_buffer_137_out, controlled_buffer_139_out, controlled_buffer_140_out,
       controlled_buffer_142_out, controlled_buffer_143_out, d_latch_1_not_q, d_latch_2_not_q,
       d_latch_3_not_q, d_latch_3_q, d_latch_4_q, d_latch_5_not_q, d_latch_6_not_q, d_latch_7_not_q,
       d_latch_8_not_q, d_latch_9_not_q, d_latch_10_not_q, d_latch_11_not_q, d_latch_12_not_q,
       d_latch_13_not_q, d_latch_14_not_q, d_latch_15_not_q, d_latch_16_not_q, d_latch_17_not_q,
       d_latch_18_not_q, d_latch_19_not_q, d_latch_20_not_q, d_latch_21_not_q, d_latch_22_not_q,
       d_latch_23_not_q, d_latch_24_not_q, d_latch_25_not_q, d_latch_26_not_q, d_latch_27_not_q,
       d_latch_28_not_q, d_latch_29_not_q, d_latch_30_not_q, d_latch_31_not_q, d_latch_32_not_q,
       d_latch_33_not_q, d_latch_34_not_q, d_latch_35_not_q, d_latch_36_not_q, d_latch_37_q,
       d_latch_38_not_q, d_latch_39_not_q, d_latch_40_not_q, d_latch_41_not_q, d_latch_42_not_q,
       d_latch_43_not_q, d_latch_44_not_q, d_latch_45_not_q, d_latch_46_not_q, d_latch_47_not_q,
       d_latch_48_not_q, d_latch_49_not_q, d_latch_50_not_q, d_latch_51_not_q, d_latch_52_not_q,
       d_latch_53_not_q, d_latch_54_not_q, d_latch_55_not_q, d_latch_56_not_q, d_latch_57_not_q,
       d_latch_58_not_q, d_latch_59_not_q, d_latch_60_not_q, d_latch_61_not_q, d_latch_62_not_q,
       d_latch_63_not_q, d_latch_64_not_q, d_latch_65_q, d_latch_66_not_q, d_latch_67_not_q,
       d_latch_68_not_q, d_latch_69_not_q, d_latch_70_not_q, d_latch_71_not_q, d_latch_72_not_q,
       d_latch_73_not_q, d_latch_74_not_q, d_latch_75_not_q, d_latch_76_not_q, d_latch_77_not_q,
       d_latch_78_not_q, d_latch_79_not_q, d_latch_80_not_q, d_latch_81_not_q, d_latch_82_not_q,
       d_latch_83_not_q, d_latch_84_not_q, d_latch_85_not_q, d_latch_86_not_q, d_latch_87_not_q,
       d_latch_88_not_q, d_latch_89_not_q, d_latch_90_not_q, d_latch_91_not_q, d_latch_92_not_q,
       d_latch_93_not_q, d_latch_94_not_q, d_latch_95_not_q, d_latch_96_not_q, d_latch_97_q,
       d_latch_98_not_q, d_latch_99_not_q, d_latch_100_not_q, d_latch_101_not_q, d_latch_102_not_q,
       d_latch_103_not_q, d_latch_104_not_q, d_latch_105_not_q, d_latch_106_not_q, d_latch_107_not_q,
       d_latch_108_not_q, d_latch_109_not_q, d_latch_110_not_q, d_latch_111_not_q, d_latch_112_not_q,
       d_latch_113_not_q, d_latch_114_not_q, d_latch_115_not_q, d_latch_116_q, d_latch_117_not_q,
       d_latch_118_not_q, d_latch_119_not_q, d_latch_120_not_q, d_latch_121_not_q, d_latch_122_not_q,
       d_latch_123_not_q, d_latch_124_not_q, d_latch_125_not_q, d_latch_126_not_q, d_latch_127_not_q,
       d_latch_128_not_q, d_latch_129_not_q, nor_1_out, nor_2_out, nor_3_out, nor_4_out, nor_5_out,
       nor_6_out, nor_7_out, not_1_out, not_2_out, not_3_out, not_4_out, not_5_out, not_6_out, not_7_out,
       not_8_out, not_9_out, not_10_out, not_11_out, not_12_out, not_13_out;

  not not_1 (not_1_out, PCLK);
  not not_2 (not_2_out, F_TA);
  not not_3 (not_3_out, F_TB);
  not not_4 (not_4_out, F_AT);
  not not_5 (not_5_out, nFO);
  not not_6 (not_6_out, TVO1);
  not not_7 (not_7_out, FH0);
  not not_8 (not_8_out, FH1);
  not not_9 (not_9_out, FH2);
  D_latch d_latch_1 (.EN(PCLK), .D(CLPB), .NOT_Q(d_latch_1_not_q));  // open: Q
  D_latch d_latch_2 (.EN(not_1_out), .D(H0), .NOT_Q(d_latch_2_not_q));  // open: Q
  D_latch d_latch_3 (.EN(PCLK), .D(THO1), .Q(d_latch_3_q), .NOT_Q(d_latch_3_not_q));
  D_latch d_latch_4 (.EN(PCLK), .D(not_4_out), .Q(d_latch_4_q));  // open: NOT_Q
  D_latch d_latch_5 (.EN(PCLK), .D(d_latch_2_not_q), .NOT_Q(d_latch_5_not_q));  // open: Q
  not not_10 (not_10_out, d_latch_5_not_q);
  nor nor_1 (nor_1_out, PCLK, not_10_out, not_3_out);
  nor nor_2 (nor_2_out, not_10_out, not_3_out);
  nor nor_3 (nor_3_out, PCLK, not_10_out, not_2_out);
  nor nor_4 (nor_4_out, PCLK, not_10_out, d_latch_4_q);
  nor nor_5 (nor_5_out, PCLK, nor_2_out, not_5_out);
  nor nor_6 (nor_6_out, PCLK, not_5_out);
  nor nor_7 (nor_7_out, nor_5_out, not_1_out, nor_6_out);
  D_latch d_latch_6 (.EN(nor_6_out), .D(d_latch_19_not_q), .NOT_Q(d_latch_6_not_q));  // open: Q
  D_latch d_latch_7 (.EN(nor_7_out), .D(d_latch_6_not_q), .NOT_Q(d_latch_7_not_q));  // open: Q
  assign controlled_buffer_1_out = FH0 ? d_latch_7_not_q : 1'bz;  // Controlled_Buffer controlled_buffer_1
  assign controlled_buffer_2_out = FH1 ? controlled_buffer_1_out : 1'bz;  // Controlled_Buffer controlled_buffer_2
  assign controlled_buffer_3_out = FH2 ? controlled_buffer_2_out : 1'bz;  // Controlled_Buffer controlled_buffer_3
  D_latch d_latch_8 (.EN(nor_6_out), .D(d_latch_7_not_q), .NOT_Q(d_latch_8_not_q));  // open: Q
  D_latch d_latch_9 (.EN(nor_7_out), .D(d_latch_8_not_q), .NOT_Q(d_latch_9_not_q));  // open: Q
  assign controlled_buffer_4_out = not_7_out ? d_latch_9_not_q : 1'bz;  // Controlled_Buffer controlled_buffer_4
  assign controlled_buffer_5_out = FH1 ? controlled_buffer_4_out : 1'bz;  // Controlled_Buffer controlled_buffer_5
  assign controlled_buffer_3_out = FH2 ? controlled_buffer_5_out : 1'bz;  // Controlled_Buffer controlled_buffer_6
  D_latch d_latch_10 (.EN(nor_4_out), .D(PD7), .NOT_Q(d_latch_10_not_q));  // open: Q
  assign controlled_buffer_7_out = d_latch_3_q ? d_latch_10_not_q : 1'bz;  // Controlled_Buffer controlled_buffer_7
  assign controlled_buffer_8_out = TVO1 ? controlled_buffer_7_out : 1'bz;  // Controlled_Buffer controlled_buffer_8
  D_latch d_latch_11 (.EN(nor_6_out), .D(d_latch_9_not_q), .NOT_Q(d_latch_11_not_q));  // open: Q
  D_latch d_latch_12 (.EN(nor_7_out), .D(d_latch_11_not_q), .NOT_Q(d_latch_12_not_q));  // open: Q
  assign controlled_buffer_9_out = FH0 ? d_latch_12_not_q : 1'bz;  // Controlled_Buffer controlled_buffer_9
  assign controlled_buffer_10_out = not_8_out ? controlled_buffer_9_out : 1'bz;  // Controlled_Buffer controlled_buffer_10
  assign controlled_buffer_3_out = FH2 ? controlled_buffer_10_out : 1'bz;  // Controlled_Buffer controlled_buffer_11
  D_latch d_latch_13 (.EN(nor_4_out), .D(PD3), .NOT_Q(d_latch_13_not_q));  // open: Q
  D_latch d_latch_14 (.EN(nor_4_out), .D(PD5), .NOT_Q(d_latch_14_not_q));  // open: Q
  assign controlled_buffer_12_out = d_latch_3_q ? d_latch_13_not_q : 1'bz;  // Controlled_Buffer controlled_buffer_12
  assign controlled_buffer_13_out = d_latch_3_not_q ? d_latch_14_not_q : 1'bz;  // Controlled_Buffer controlled_buffer_13
  assign controlled_buffer_8_out = TVO1 ? controlled_buffer_13_out : 1'bz;  // Controlled_Buffer controlled_buffer_14
  assign controlled_buffer_8_out = not_6_out ? controlled_buffer_12_out : 1'bz;  // Controlled_Buffer controlled_buffer_15
  D_latch d_latch_15 (.EN(nor_1_out), .D(controlled_buffer_8_out), .NOT_Q(d_latch_15_not_q));  // open: Q
  D_latch d_latch_16 (.EN(nor_6_out), .D(d_latch_12_not_q), .NOT_Q(d_latch_16_not_q));  // open: Q
  D_latch d_latch_17 (.EN(nor_7_out), .D(d_latch_16_not_q), .NOT_Q(d_latch_17_not_q));  // open: Q
  D_latch d_latch_18 (.EN(nor_4_out), .D(PD1), .NOT_Q(d_latch_18_not_q));  // open: Q
  assign controlled_buffer_16_out = d_latch_3_not_q ? d_latch_18_not_q : 1'bz;  // Controlled_Buffer controlled_buffer_16
  assign controlled_buffer_8_out = not_6_out ? controlled_buffer_16_out : 1'bz;  // Controlled_Buffer controlled_buffer_17
  D_latch d_latch_19 (.EN(nor_7_out), .D(d_latch_15_not_q), .NOT_Q(d_latch_19_not_q));  // open: Q
  assign controlled_buffer_18_out = not_7_out ? d_latch_17_not_q : 1'bz;  // Controlled_Buffer controlled_buffer_18
  assign controlled_buffer_19_out = not_8_out ? controlled_buffer_18_out : 1'bz;  // Controlled_Buffer controlled_buffer_19
  assign controlled_buffer_3_out = FH2 ? controlled_buffer_19_out : 1'bz;  // Controlled_Buffer controlled_buffer_20
  D_latch d_latch_20 (.EN(nor_4_out), .D(PD6), .NOT_Q(d_latch_20_not_q));  // open: Q
  assign controlled_buffer_21_out = d_latch_3_q ? d_latch_20_not_q : 1'bz;  // Controlled_Buffer controlled_buffer_21
  assign controlled_buffer_22_out = TVO1 ? controlled_buffer_21_out : 1'bz;  // Controlled_Buffer controlled_buffer_22
  D_latch d_latch_21 (.EN(nor_6_out), .D(d_latch_17_not_q), .NOT_Q(d_latch_21_not_q));  // open: Q
  D_latch d_latch_22 (.EN(nor_7_out), .D(d_latch_21_not_q), .NOT_Q(d_latch_22_not_q));  // open: Q
  assign controlled_buffer_23_out = FH0 ? d_latch_22_not_q : 1'bz;  // Controlled_Buffer controlled_buffer_23
  assign controlled_buffer_24_out = FH1 ? controlled_buffer_23_out : 1'bz;  // Controlled_Buffer controlled_buffer_24
  assign controlled_buffer_3_out = not_9_out ? controlled_buffer_24_out : 1'bz;  // Controlled_Buffer controlled_buffer_25
  D_latch d_latch_23 (.EN(nor_4_out), .D(PD4), .NOT_Q(d_latch_23_not_q));  // open: Q
  assign controlled_buffer_26_out = d_latch_3_not_q ? d_latch_23_not_q : 1'bz;  // Controlled_Buffer controlled_buffer_26
  assign controlled_buffer_22_out = TVO1 ? controlled_buffer_26_out : 1'bz;  // Controlled_Buffer controlled_buffer_27
  D_latch d_latch_24 (.EN(nor_1_out), .D(controlled_buffer_22_out), .NOT_Q(d_latch_24_not_q));  // open: Q
  D_latch d_latch_25 (.EN(nor_6_out), .D(d_latch_22_not_q), .NOT_Q(d_latch_25_not_q));  // open: Q
  D_latch d_latch_26 (.EN(nor_7_out), .D(d_latch_25_not_q), .NOT_Q(d_latch_26_not_q));  // open: Q
  assign controlled_buffer_28_out = not_7_out ? d_latch_26_not_q : 1'bz;  // Controlled_Buffer controlled_buffer_28
  assign controlled_buffer_29_out = FH1 ? controlled_buffer_28_out : 1'bz;  // Controlled_Buffer controlled_buffer_29
  assign controlled_buffer_3_out = not_9_out ? controlled_buffer_29_out : 1'bz;  // Controlled_Buffer controlled_buffer_30
  D_latch d_latch_27 (.EN(nor_4_out), .D(PD2), .NOT_Q(d_latch_27_not_q));  // open: Q
  assign controlled_buffer_31_out = d_latch_3_q ? d_latch_27_not_q : 1'bz;  // Controlled_Buffer controlled_buffer_31
  assign controlled_buffer_22_out = not_6_out ? controlled_buffer_31_out : 1'bz;  // Controlled_Buffer controlled_buffer_32
  D_latch d_latch_28 (.EN(nor_7_out), .D(d_latch_24_not_q), .NOT_Q(d_latch_28_not_q));  // open: Q
  D_latch d_latch_29 (.EN(nor_6_out), .D(d_latch_26_not_q), .NOT_Q(d_latch_29_not_q));  // open: Q
  D_latch d_latch_30 (.EN(nor_7_out), .D(d_latch_29_not_q), .NOT_Q(d_latch_30_not_q));  // open: Q
  assign controlled_buffer_33_out = FH0 ? d_latch_30_not_q : 1'bz;  // Controlled_Buffer controlled_buffer_33
  assign controlled_buffer_34_out = not_8_out ? controlled_buffer_33_out : 1'bz;  // Controlled_Buffer controlled_buffer_34
  assign controlled_buffer_3_out = not_9_out ? controlled_buffer_34_out : 1'bz;  // Controlled_Buffer controlled_buffer_35
  D_latch d_latch_31 (.EN(nor_4_out), .D(PD0), .NOT_Q(d_latch_31_not_q));  // open: Q
  assign controlled_buffer_36_out = d_latch_3_not_q ? d_latch_31_not_q : 1'bz;  // Controlled_Buffer controlled_buffer_36
  assign controlled_buffer_22_out = not_6_out ? controlled_buffer_36_out : 1'bz;  // Controlled_Buffer controlled_buffer_37
  D_latch d_latch_32 (.EN(nor_6_out), .D(d_latch_30_not_q), .NOT_Q(d_latch_32_not_q));  // open: Q
  D_latch d_latch_33 (.EN(nor_7_out), .D(d_latch_32_not_q), .NOT_Q(d_latch_33_not_q));  // open: Q
  assign controlled_buffer_38_out = not_7_out ? d_latch_33_not_q : 1'bz;  // Controlled_Buffer controlled_buffer_38
  assign controlled_buffer_39_out = not_8_out ? controlled_buffer_38_out : 1'bz;  // Controlled_Buffer controlled_buffer_39
  assign controlled_buffer_3_out = not_9_out ? controlled_buffer_39_out : 1'bz;  // Controlled_Buffer controlled_buffer_40
  assign controlled_buffer_41_out = nor_1_out ? PD0 : 1'bz;  // Controlled_Buffer controlled_buffer_41
  assign controlled_buffer_41_out = nor_5_out ? 1'b1 : 1'bz;  // Controlled_Buffer controlled_buffer_42
  D_latch d_latch_34 (.EN(not_1_out), .D(not_11_out), .NOT_Q(d_latch_34_not_q));  // open: Q
  not not_11 (not_11_out, controlled_buffer_3_out);
  D_latch d_latch_35 (.EN(1'b1), .D(controlled_buffer_41_out), .NOT_Q(d_latch_35_not_q));  // open: Q
  D_latch d_latch_36 (.EN(nor_7_out), .D(d_latch_35_not_q), .NOT_Q(d_latch_36_not_q));  // open: Q
  D_latch d_latch_37 (.EN(PCLK), .D(d_latch_34_not_q), .Q(d_latch_37_q));  // open: NOT_Q
  assign controlled_buffer_43_out = nor_1_out ? PD1 : 1'bz;  // Controlled_Buffer controlled_buffer_43
  assign controlled_buffer_43_out = nor_5_out ? d_latch_36_not_q : 1'bz;  // Controlled_Buffer controlled_buffer_44
  D_latch d_latch_38 (.EN(nor_6_out), .D(d_latch_28_not_q), .NOT_Q(d_latch_38_not_q));  // open: Q
  D_latch d_latch_39 (.EN(nor_7_out), .D(d_latch_38_not_q), .NOT_Q(d_latch_39_not_q));  // open: Q
  assign controlled_buffer_45_out = FH0 ? d_latch_39_not_q : 1'bz;  // Controlled_Buffer controlled_buffer_45
  assign controlled_buffer_46_out = FH1 ? controlled_buffer_45_out : 1'bz;  // Controlled_Buffer controlled_buffer_46
  assign controlled_buffer_47_out = FH2 ? controlled_buffer_46_out : 1'bz;  // Controlled_Buffer controlled_buffer_47
  D_latch d_latch_40 (.EN(1'b1), .D(controlled_buffer_43_out), .NOT_Q(d_latch_40_not_q));  // open: Q
  D_latch d_latch_41 (.EN(nor_7_out), .D(d_latch_40_not_q), .NOT_Q(d_latch_41_not_q));  // open: Q
  D_latch d_latch_42 (.EN(nor_6_out), .D(d_latch_39_not_q), .NOT_Q(d_latch_42_not_q));  // open: Q
  D_latch d_latch_43 (.EN(nor_7_out), .D(d_latch_42_not_q), .NOT_Q(d_latch_43_not_q));  // open: Q
  assign controlled_buffer_48_out = not_7_out ? d_latch_43_not_q : 1'bz;  // Controlled_Buffer controlled_buffer_48
  assign controlled_buffer_49_out = FH1 ? controlled_buffer_48_out : 1'bz;  // Controlled_Buffer controlled_buffer_49
  assign controlled_buffer_47_out = FH2 ? controlled_buffer_49_out : 1'bz;  // Controlled_Buffer controlled_buffer_50
  nor nor_8 (BGC3, d_latch_37_q, d_latch_1_not_q);
  assign controlled_buffer_51_out = nor_1_out ? PD2 : 1'bz;  // Controlled_Buffer controlled_buffer_51
  assign controlled_buffer_51_out = nor_5_out ? d_latch_41_not_q : 1'bz;  // Controlled_Buffer controlled_buffer_52
  D_latch d_latch_44 (.EN(nor_6_out), .D(d_latch_43_not_q), .NOT_Q(d_latch_44_not_q));  // open: Q
  D_latch d_latch_45 (.EN(nor_7_out), .D(d_latch_44_not_q), .NOT_Q(d_latch_45_not_q));  // open: Q
  assign controlled_buffer_53_out = FH0 ? d_latch_45_not_q : 1'bz;  // Controlled_Buffer controlled_buffer_53
  assign controlled_buffer_54_out = not_8_out ? controlled_buffer_53_out : 1'bz;  // Controlled_Buffer controlled_buffer_54
  assign controlled_buffer_47_out = FH2 ? controlled_buffer_54_out : 1'bz;  // Controlled_Buffer controlled_buffer_55
  D_latch d_latch_46 (.EN(1'b1), .D(controlled_buffer_51_out), .NOT_Q(d_latch_46_not_q));  // open: Q
  D_latch d_latch_47 (.EN(nor_7_out), .D(d_latch_46_not_q), .NOT_Q(d_latch_47_not_q));  // open: Q
  D_latch d_latch_48 (.EN(nor_6_out), .D(d_latch_45_not_q), .NOT_Q(d_latch_48_not_q));  // open: Q
  D_latch d_latch_49 (.EN(nor_7_out), .D(d_latch_48_not_q), .NOT_Q(d_latch_49_not_q));  // open: Q
  assign controlled_buffer_56_out = nor_1_out ? PD3 : 1'bz;  // Controlled_Buffer controlled_buffer_56
  assign controlled_buffer_56_out = nor_5_out ? d_latch_47_not_q : 1'bz;  // Controlled_Buffer controlled_buffer_57
  assign controlled_buffer_58_out = not_7_out ? d_latch_49_not_q : 1'bz;  // Controlled_Buffer controlled_buffer_58
  assign controlled_buffer_59_out = not_8_out ? controlled_buffer_58_out : 1'bz;  // Controlled_Buffer controlled_buffer_59
  assign controlled_buffer_47_out = FH2 ? controlled_buffer_59_out : 1'bz;  // Controlled_Buffer controlled_buffer_60
  D_latch d_latch_50 (.EN(1'b1), .D(controlled_buffer_56_out), .NOT_Q(d_latch_50_not_q));  // open: Q
  D_latch d_latch_51 (.EN(nor_7_out), .D(d_latch_50_not_q), .NOT_Q(d_latch_51_not_q));  // open: Q
  D_latch d_latch_52 (.EN(nor_6_out), .D(d_latch_49_not_q), .NOT_Q(d_latch_52_not_q));  // open: Q
  D_latch d_latch_53 (.EN(nor_7_out), .D(d_latch_52_not_q), .NOT_Q(d_latch_53_not_q));  // open: Q
  assign controlled_buffer_61_out = FH0 ? d_latch_53_not_q : 1'bz;  // Controlled_Buffer controlled_buffer_61
  assign controlled_buffer_62_out = FH1 ? controlled_buffer_61_out : 1'bz;  // Controlled_Buffer controlled_buffer_62
  assign controlled_buffer_47_out = not_9_out ? controlled_buffer_62_out : 1'bz;  // Controlled_Buffer controlled_buffer_63
  assign controlled_buffer_64_out = nor_1_out ? PD4 : 1'bz;  // Controlled_Buffer controlled_buffer_64
  assign controlled_buffer_64_out = nor_5_out ? d_latch_51_not_q : 1'bz;  // Controlled_Buffer controlled_buffer_65
  D_latch d_latch_54 (.EN(nor_6_out), .D(d_latch_53_not_q), .NOT_Q(d_latch_54_not_q));  // open: Q
  D_latch d_latch_55 (.EN(nor_7_out), .D(d_latch_54_not_q), .NOT_Q(d_latch_55_not_q));  // open: Q
  assign controlled_buffer_66_out = not_7_out ? d_latch_55_not_q : 1'bz;  // Controlled_Buffer controlled_buffer_66
  assign controlled_buffer_67_out = FH1 ? controlled_buffer_66_out : 1'bz;  // Controlled_Buffer controlled_buffer_67
  assign controlled_buffer_47_out = not_9_out ? controlled_buffer_67_out : 1'bz;  // Controlled_Buffer controlled_buffer_68
  D_latch d_latch_56 (.EN(1'b1), .D(controlled_buffer_64_out), .NOT_Q(d_latch_56_not_q));  // open: Q
  D_latch d_latch_57 (.EN(nor_7_out), .D(d_latch_56_not_q), .NOT_Q(d_latch_57_not_q));  // open: Q
  D_latch d_latch_58 (.EN(nor_6_out), .D(d_latch_55_not_q), .NOT_Q(d_latch_58_not_q));  // open: Q
  D_latch d_latch_59 (.EN(nor_7_out), .D(d_latch_58_not_q), .NOT_Q(d_latch_59_not_q));  // open: Q
  assign controlled_buffer_69_out = FH0 ? d_latch_59_not_q : 1'bz;  // Controlled_Buffer controlled_buffer_69
  assign controlled_buffer_70_out = not_8_out ? controlled_buffer_69_out : 1'bz;  // Controlled_Buffer controlled_buffer_70
  assign controlled_buffer_47_out = not_9_out ? controlled_buffer_70_out : 1'bz;  // Controlled_Buffer controlled_buffer_71
  assign controlled_buffer_72_out = nor_5_out ? d_latch_57_not_q : 1'bz;  // Controlled_Buffer controlled_buffer_72
  D_latch d_latch_60 (.EN(nor_6_out), .D(d_latch_59_not_q), .NOT_Q(d_latch_60_not_q));  // open: Q
  D_latch d_latch_61 (.EN(nor_7_out), .D(d_latch_60_not_q), .NOT_Q(d_latch_61_not_q));  // open: Q
  assign controlled_buffer_72_out = nor_1_out ? PD5 : 1'bz;  // Controlled_Buffer controlled_buffer_73
  assign controlled_buffer_74_out = not_7_out ? d_latch_61_not_q : 1'bz;  // Controlled_Buffer controlled_buffer_74
  assign controlled_buffer_75_out = not_8_out ? controlled_buffer_74_out : 1'bz;  // Controlled_Buffer controlled_buffer_75
  assign controlled_buffer_47_out = not_9_out ? controlled_buffer_75_out : 1'bz;  // Controlled_Buffer controlled_buffer_76
  not not_12 (not_12_out, controlled_buffer_47_out);
  D_latch d_latch_62 (.EN(1'b1), .D(controlled_buffer_72_out), .NOT_Q(d_latch_62_not_q));  // open: Q
  assign controlled_buffer_77_out = nor_5_out ? d_latch_63_not_q : 1'bz;  // Controlled_Buffer controlled_buffer_77
  D_latch d_latch_63 (.EN(nor_7_out), .D(d_latch_62_not_q), .NOT_Q(d_latch_63_not_q));  // open: Q
  D_latch d_latch_64 (.EN(not_1_out), .D(not_12_out), .NOT_Q(d_latch_64_not_q));  // open: Q
  assign controlled_buffer_77_out = nor_1_out ? PD6 : 1'bz;  // Controlled_Buffer controlled_buffer_78
  D_latch d_latch_65 (.EN(PCLK), .D(d_latch_64_not_q), .Q(d_latch_65_q));  // open: NOT_Q
  D_latch d_latch_66 (.EN(1'b1), .D(controlled_buffer_77_out), .NOT_Q(d_latch_66_not_q));  // open: Q
  D_latch d_latch_67 (.EN(nor_7_out), .D(d_latch_66_not_q), .NOT_Q(d_latch_67_not_q));  // open: Q
  D_latch d_latch_68 (.EN(nor_6_out), .D(d_latch_73_not_q), .NOT_Q(d_latch_68_not_q));  // open: Q
  D_latch d_latch_69 (.EN(nor_7_out), .D(d_latch_68_not_q), .NOT_Q(d_latch_69_not_q));  // open: Q
  assign controlled_buffer_79_out = FH0 ? d_latch_69_not_q : 1'bz;  // Controlled_Buffer controlled_buffer_79
  assign controlled_buffer_80_out = FH1 ? controlled_buffer_79_out : 1'bz;  // Controlled_Buffer controlled_buffer_80
  assign controlled_buffer_81_out = FH2 ? controlled_buffer_80_out : 1'bz;  // Controlled_Buffer controlled_buffer_81
  nor nor_9 (BGC2, d_latch_65_q, d_latch_1_not_q);
  assign controlled_buffer_82_out = nor_1_out ? PD7 : 1'bz;  // Controlled_Buffer controlled_buffer_82
  assign controlled_buffer_82_out = nor_5_out ? d_latch_67_not_q : 1'bz;  // Controlled_Buffer controlled_buffer_83
  D_latch d_latch_70 (.EN(nor_6_out), .D(d_latch_69_not_q), .NOT_Q(d_latch_70_not_q));  // open: Q
  D_latch d_latch_71 (.EN(nor_7_out), .D(d_latch_70_not_q), .NOT_Q(d_latch_71_not_q));  // open: Q
  assign controlled_buffer_84_out = not_7_out ? d_latch_71_not_q : 1'bz;  // Controlled_Buffer controlled_buffer_84
  assign controlled_buffer_85_out = FH1 ? controlled_buffer_84_out : 1'bz;  // Controlled_Buffer controlled_buffer_85
  assign controlled_buffer_81_out = FH2 ? controlled_buffer_85_out : 1'bz;  // Controlled_Buffer controlled_buffer_86
  D_latch d_latch_72 (.EN(1'b1), .D(controlled_buffer_82_out), .NOT_Q(d_latch_72_not_q));  // open: Q
  D_latch d_latch_73 (.EN(nor_7_out), .D(d_latch_72_not_q), .NOT_Q(d_latch_73_not_q));  // open: Q
  D_latch d_latch_74 (.EN(nor_6_out), .D(d_latch_71_not_q), .NOT_Q(d_latch_74_not_q));  // open: Q
  D_latch d_latch_75 (.EN(nor_7_out), .D(d_latch_74_not_q), .NOT_Q(d_latch_75_not_q));  // open: Q
  D_latch d_latch_76 (.EN(nor_3_out), .D(PD0), .NOT_Q(d_latch_76_not_q));  // open: Q
  assign controlled_buffer_87_out = FH0 ? d_latch_75_not_q : 1'bz;  // Controlled_Buffer controlled_buffer_87
  assign controlled_buffer_88_out = not_8_out ? controlled_buffer_87_out : 1'bz;  // Controlled_Buffer controlled_buffer_88
  assign controlled_buffer_81_out = FH2 ? controlled_buffer_88_out : 1'bz;  // Controlled_Buffer controlled_buffer_89
  assign controlled_buffer_90_out = nor_1_out ? d_latch_76_not_q : 1'bz;  // Controlled_Buffer controlled_buffer_90
  assign controlled_buffer_90_out = nor_5_out ? 1'b1 : 1'bz;  // Controlled_Buffer controlled_buffer_91
  D_latch d_latch_77 (.EN(nor_6_out), .D(d_latch_75_not_q), .NOT_Q(d_latch_77_not_q));  // open: Q
  D_latch d_latch_78 (.EN(nor_7_out), .D(d_latch_77_not_q), .NOT_Q(d_latch_78_not_q));  // open: Q
  assign controlled_buffer_92_out = not_7_out ? d_latch_78_not_q : 1'bz;  // Controlled_Buffer controlled_buffer_92
  assign controlled_buffer_93_out = not_8_out ? controlled_buffer_92_out : 1'bz;  // Controlled_Buffer controlled_buffer_93
  assign controlled_buffer_81_out = FH2 ? controlled_buffer_93_out : 1'bz;  // Controlled_Buffer controlled_buffer_94
  D_latch d_latch_79 (.EN(1'b1), .D(controlled_buffer_90_out), .NOT_Q(d_latch_79_not_q));  // open: Q
  D_latch d_latch_80 (.EN(nor_7_out), .D(d_latch_79_not_q), .NOT_Q(d_latch_80_not_q));  // open: Q
  D_latch d_latch_81 (.EN(nor_6_out), .D(d_latch_78_not_q), .NOT_Q(d_latch_81_not_q));  // open: Q
  D_latch d_latch_82 (.EN(nor_7_out), .D(d_latch_81_not_q), .NOT_Q(d_latch_82_not_q));  // open: Q
  assign controlled_buffer_95_out = FH0 ? d_latch_82_not_q : 1'bz;  // Controlled_Buffer controlled_buffer_95
  assign controlled_buffer_96_out = FH1 ? controlled_buffer_95_out : 1'bz;  // Controlled_Buffer controlled_buffer_96
  assign controlled_buffer_81_out = not_9_out ? controlled_buffer_96_out : 1'bz;  // Controlled_Buffer controlled_buffer_97
  D_latch d_latch_83 (.EN(nor_3_out), .D(PD1), .NOT_Q(d_latch_83_not_q));  // open: Q
  assign controlled_buffer_98_out = nor_1_out ? d_latch_83_not_q : 1'bz;  // Controlled_Buffer controlled_buffer_98
  assign controlled_buffer_98_out = nor_5_out ? d_latch_80_not_q : 1'bz;  // Controlled_Buffer controlled_buffer_99
  D_latch d_latch_84 (.EN(nor_6_out), .D(d_latch_82_not_q), .NOT_Q(d_latch_84_not_q));  // open: Q
  D_latch d_latch_85 (.EN(nor_7_out), .D(d_latch_84_not_q), .NOT_Q(d_latch_85_not_q));  // open: Q
  assign controlled_buffer_100_out = not_7_out ? d_latch_85_not_q : 1'bz;  // Controlled_Buffer controlled_buffer_100
  assign controlled_buffer_101_out = FH1 ? controlled_buffer_100_out : 1'bz;  // Controlled_Buffer controlled_buffer_101
  assign controlled_buffer_81_out = not_9_out ? controlled_buffer_101_out : 1'bz;  // Controlled_Buffer controlled_buffer_102
  D_latch d_latch_86 (.EN(1'b1), .D(controlled_buffer_98_out), .NOT_Q(d_latch_86_not_q));  // open: Q
  D_latch d_latch_87 (.EN(nor_7_out), .D(d_latch_86_not_q), .NOT_Q(d_latch_87_not_q));  // open: Q
  D_latch d_latch_88 (.EN(nor_6_out), .D(d_latch_85_not_q), .NOT_Q(d_latch_88_not_q));  // open: Q
  D_latch d_latch_89 (.EN(nor_7_out), .D(d_latch_88_not_q), .NOT_Q(d_latch_89_not_q));  // open: Q
  D_latch d_latch_90 (.EN(nor_3_out), .D(PD2), .NOT_Q(d_latch_90_not_q));  // open: Q
  assign controlled_buffer_103_out = nor_5_out ? d_latch_87_not_q : 1'bz;  // Controlled_Buffer controlled_buffer_103
  assign controlled_buffer_104_out = FH0 ? d_latch_89_not_q : 1'bz;  // Controlled_Buffer controlled_buffer_104
  assign controlled_buffer_105_out = not_8_out ? controlled_buffer_104_out : 1'bz;  // Controlled_Buffer controlled_buffer_105
  assign controlled_buffer_81_out = not_9_out ? controlled_buffer_105_out : 1'bz;  // Controlled_Buffer controlled_buffer_106
  assign controlled_buffer_103_out = nor_1_out ? d_latch_90_not_q : 1'bz;  // Controlled_Buffer controlled_buffer_107
  D_latch d_latch_91 (.EN(nor_6_out), .D(d_latch_89_not_q), .NOT_Q(d_latch_91_not_q));  // open: Q
  D_latch d_latch_92 (.EN(nor_7_out), .D(d_latch_91_not_q), .NOT_Q(d_latch_92_not_q));  // open: Q
  assign controlled_buffer_108_out = not_7_out ? d_latch_92_not_q : 1'bz;  // Controlled_Buffer controlled_buffer_108
  assign controlled_buffer_109_out = not_8_out ? controlled_buffer_108_out : 1'bz;  // Controlled_Buffer controlled_buffer_109
  assign controlled_buffer_81_out = not_9_out ? controlled_buffer_109_out : 1'bz;  // Controlled_Buffer controlled_buffer_110
  D_latch d_latch_93 (.EN(nor_3_out), .D(PD3), .NOT_Q(d_latch_93_not_q));  // open: Q
  D_latch d_latch_94 (.EN(1'b1), .D(controlled_buffer_103_out), .NOT_Q(d_latch_94_not_q));  // open: Q
  assign controlled_buffer_111_out = nor_5_out ? d_latch_95_not_q : 1'bz;  // Controlled_Buffer controlled_buffer_111
  D_latch d_latch_95 (.EN(nor_7_out), .D(d_latch_94_not_q), .NOT_Q(d_latch_95_not_q));  // open: Q
  D_latch d_latch_96 (.EN(not_1_out), .D(controlled_buffer_81_out), .NOT_Q(d_latch_96_not_q));  // open: Q
  assign controlled_buffer_111_out = nor_1_out ? d_latch_93_not_q : 1'bz;  // Controlled_Buffer controlled_buffer_112
  D_latch d_latch_97 (.EN(PCLK), .D(d_latch_96_not_q), .Q(d_latch_97_q));  // open: NOT_Q
  D_latch d_latch_98 (.EN(nor_3_out), .D(PD4), .NOT_Q(d_latch_98_not_q));  // open: Q
  D_latch d_latch_99 (.EN(1'b1), .D(controlled_buffer_111_out), .NOT_Q(d_latch_99_not_q));  // open: Q
  D_latch d_latch_100 (.EN(nor_7_out), .D(d_latch_99_not_q), .NOT_Q(d_latch_100_not_q));  // open: Q
  D_latch d_latch_101 (.EN(nor_6_out), .D(d_latch_127_not_q), .NOT_Q(d_latch_101_not_q));  // open: Q
  D_latch d_latch_102 (.EN(nor_7_out), .D(d_latch_101_not_q), .NOT_Q(d_latch_102_not_q));  // open: Q
  assign controlled_buffer_113_out = FH0 ? d_latch_102_not_q : 1'bz;  // Controlled_Buffer controlled_buffer_113
  assign controlled_buffer_114_out = FH1 ? controlled_buffer_113_out : 1'bz;  // Controlled_Buffer controlled_buffer_114
  assign controlled_buffer_115_out = FH2 ? controlled_buffer_114_out : 1'bz;  // Controlled_Buffer controlled_buffer_115
  assign controlled_buffer_116_out = nor_1_out ? d_latch_98_not_q : 1'bz;  // Controlled_Buffer controlled_buffer_116
  assign controlled_buffer_116_out = nor_5_out ? d_latch_100_not_q : 1'bz;  // Controlled_Buffer controlled_buffer_117
  D_latch d_latch_103 (.EN(nor_6_out), .D(d_latch_102_not_q), .NOT_Q(d_latch_103_not_q));  // open: Q
  D_latch d_latch_104 (.EN(nor_7_out), .D(d_latch_103_not_q), .NOT_Q(d_latch_104_not_q));  // open: Q
  assign controlled_buffer_118_out = not_7_out ? d_latch_104_not_q : 1'bz;  // Controlled_Buffer controlled_buffer_118
  assign controlled_buffer_119_out = FH1 ? controlled_buffer_118_out : 1'bz;  // Controlled_Buffer controlled_buffer_119
  assign controlled_buffer_115_out = FH2 ? controlled_buffer_119_out : 1'bz;  // Controlled_Buffer controlled_buffer_120
  nor nor_10 (BGC1, d_latch_97_q, d_latch_1_not_q);
  D_latch d_latch_105 (.EN(nor_3_out), .D(PD5), .NOT_Q(d_latch_105_not_q));  // open: Q
  D_latch d_latch_106 (.EN(1'b1), .D(controlled_buffer_116_out), .NOT_Q(d_latch_106_not_q));  // open: Q
  D_latch d_latch_107 (.EN(nor_7_out), .D(d_latch_106_not_q), .NOT_Q(d_latch_107_not_q));  // open: Q
  D_latch d_latch_108 (.EN(nor_6_out), .D(d_latch_104_not_q), .NOT_Q(d_latch_108_not_q));  // open: Q
  D_latch d_latch_109 (.EN(nor_7_out), .D(d_latch_108_not_q), .NOT_Q(d_latch_109_not_q));  // open: Q
  not not_13 (not_13_out, controlled_buffer_115_out);
  assign controlled_buffer_121_out = nor_1_out ? d_latch_105_not_q : 1'bz;  // Controlled_Buffer controlled_buffer_121
  assign controlled_buffer_121_out = nor_5_out ? d_latch_107_not_q : 1'bz;  // Controlled_Buffer controlled_buffer_122
  assign controlled_buffer_123_out = FH0 ? d_latch_109_not_q : 1'bz;  // Controlled_Buffer controlled_buffer_123
  assign controlled_buffer_124_out = not_8_out ? controlled_buffer_123_out : 1'bz;  // Controlled_Buffer controlled_buffer_124
  assign controlled_buffer_115_out = FH2 ? controlled_buffer_124_out : 1'bz;  // Controlled_Buffer controlled_buffer_125
  D_latch d_latch_110 (.EN(not_1_out), .D(not_13_out), .NOT_Q(d_latch_110_not_q));  // open: Q
  D_latch d_latch_111 (.EN(nor_3_out), .D(PD6), .NOT_Q(d_latch_111_not_q));  // open: Q
  D_latch d_latch_112 (.EN(1'b1), .D(controlled_buffer_121_out), .NOT_Q(d_latch_112_not_q));  // open: Q
  D_latch d_latch_113 (.EN(nor_7_out), .D(d_latch_112_not_q), .NOT_Q(d_latch_113_not_q));  // open: Q
  D_latch d_latch_114 (.EN(nor_6_out), .D(d_latch_109_not_q), .NOT_Q(d_latch_114_not_q));  // open: Q
  D_latch d_latch_115 (.EN(nor_7_out), .D(d_latch_114_not_q), .NOT_Q(d_latch_115_not_q));  // open: Q
  assign controlled_buffer_126_out = not_7_out ? d_latch_115_not_q : 1'bz;  // Controlled_Buffer controlled_buffer_126
  assign controlled_buffer_127_out = not_8_out ? controlled_buffer_126_out : 1'bz;  // Controlled_Buffer controlled_buffer_127
  assign controlled_buffer_115_out = FH2 ? controlled_buffer_127_out : 1'bz;  // Controlled_Buffer controlled_buffer_128
  D_latch d_latch_116 (.EN(PCLK), .D(d_latch_110_not_q), .Q(d_latch_116_q));  // open: NOT_Q
  assign controlled_buffer_129_out = nor_1_out ? d_latch_111_not_q : 1'bz;  // Controlled_Buffer controlled_buffer_129
  assign controlled_buffer_129_out = nor_5_out ? d_latch_113_not_q : 1'bz;  // Controlled_Buffer controlled_buffer_130
  D_latch d_latch_117 (.EN(nor_6_out), .D(d_latch_115_not_q), .NOT_Q(d_latch_117_not_q));  // open: Q
  D_latch d_latch_118 (.EN(nor_7_out), .D(d_latch_117_not_q), .NOT_Q(d_latch_118_not_q));  // open: Q
  assign controlled_buffer_131_out = FH0 ? d_latch_118_not_q : 1'bz;  // Controlled_Buffer controlled_buffer_131
  assign controlled_buffer_132_out = FH1 ? controlled_buffer_131_out : 1'bz;  // Controlled_Buffer controlled_buffer_132
  assign controlled_buffer_115_out = not_9_out ? controlled_buffer_132_out : 1'bz;  // Controlled_Buffer controlled_buffer_133
  nor nor_11 (BGC0, d_latch_116_q, d_latch_1_not_q);
  D_latch d_latch_119 (.EN(nor_3_out), .D(PD7), .NOT_Q(d_latch_119_not_q));  // open: Q
  D_latch d_latch_120 (.EN(1'b1), .D(controlled_buffer_129_out), .NOT_Q(d_latch_120_not_q));  // open: Q
  D_latch d_latch_121 (.EN(nor_7_out), .D(d_latch_120_not_q), .NOT_Q(d_latch_121_not_q));  // open: Q
  D_latch d_latch_122 (.EN(nor_6_out), .D(d_latch_118_not_q), .NOT_Q(d_latch_122_not_q));  // open: Q
  D_latch d_latch_123 (.EN(nor_7_out), .D(d_latch_122_not_q), .NOT_Q(d_latch_123_not_q));  // open: Q
  assign controlled_buffer_134_out = not_7_out ? d_latch_123_not_q : 1'bz;  // Controlled_Buffer controlled_buffer_134
  assign controlled_buffer_135_out = FH1 ? controlled_buffer_134_out : 1'bz;  // Controlled_Buffer controlled_buffer_135
  assign controlled_buffer_115_out = not_9_out ? controlled_buffer_135_out : 1'bz;  // Controlled_Buffer controlled_buffer_136
  assign controlled_buffer_137_out = nor_1_out ? d_latch_119_not_q : 1'bz;  // Controlled_Buffer controlled_buffer_137
  assign controlled_buffer_137_out = nor_5_out ? d_latch_121_not_q : 1'bz;  // Controlled_Buffer controlled_buffer_138
  D_latch d_latch_124 (.EN(nor_6_out), .D(d_latch_123_not_q), .NOT_Q(d_latch_124_not_q));  // open: Q
  D_latch d_latch_125 (.EN(nor_7_out), .D(d_latch_124_not_q), .NOT_Q(d_latch_125_not_q));  // open: Q
  D_latch d_latch_126 (.EN(1'b1), .D(controlled_buffer_137_out), .NOT_Q(d_latch_126_not_q));  // open: Q
  D_latch d_latch_127 (.EN(nor_7_out), .D(d_latch_126_not_q), .NOT_Q(d_latch_127_not_q));  // open: Q
  assign controlled_buffer_139_out = FH0 ? d_latch_125_not_q : 1'bz;  // Controlled_Buffer controlled_buffer_139
  assign controlled_buffer_140_out = not_8_out ? controlled_buffer_139_out : 1'bz;  // Controlled_Buffer controlled_buffer_140
  assign controlled_buffer_115_out = not_9_out ? controlled_buffer_140_out : 1'bz;  // Controlled_Buffer controlled_buffer_141
  D_latch d_latch_128 (.EN(nor_6_out), .D(d_latch_125_not_q), .NOT_Q(d_latch_128_not_q));  // open: Q
  D_latch d_latch_129 (.EN(nor_7_out), .D(d_latch_128_not_q), .NOT_Q(d_latch_129_not_q));  // open: Q
  assign controlled_buffer_142_out = not_7_out ? d_latch_129_not_q : 1'bz;  // Controlled_Buffer controlled_buffer_142
  assign controlled_buffer_143_out = not_8_out ? controlled_buffer_142_out : 1'bz;  // Controlled_Buffer controlled_buffer_143
  assign controlled_buffer_115_out = not_9_out ? controlled_buffer_143_out : 1'bz;  // Controlled_Buffer controlled_buffer_144

  // Notes on the sheet:
  //   /PCLK
  //   PCLK
  //   VO1
  //   /VO1
  //   HO1
  //   /HO1
  //   /H0''
  //   PD/SR
  //   PD/SEL
  //   SRLOAD
  //   STEP
  //   STEP2
  //   NEXT
  //   SRLOAD
  //   STEP
  //   NEXT
  //   PCLK
  //   /PCLK
  //   PD/SR
endmodule
