// Logisim project 2C04 PPU RGB OUT.circ as structural Verilog: 8 circuits, main circuit main
module main (
);

  wire clock_1_out, counter_1_carry, rgb_out_1_b, rgb_out_1_g, rgb_out_1_out_14, rgb_out_1_out_15,
       rgb_out_1_out_16, rgb_out_1_out_17, rgb_out_1_out_18, rgb_out_1_out_19, rgb_out_1_out_20,
       rgb_out_1_out_22, rgb_out_1_out_23, rgb_out_1_out_24, rgb_out_1_out_25, rgb_out_1_out_26,
       rgb_out_1_out_27, rgb_out_1_out_28, rgb_out_1_out_30, rgb_out_1_out_31, rgb_out_1_out_32,
       rgb_out_1_out_33, rgb_out_1_out_34, rgb_out_1_out_35, rgb_out_1_out_36, rgb_out_1_r, rgb_out_1_sync_2;
  wire [5:0] counter_1_q;

  Counter #(.width(6), .max('h3f)) counter_1 (
    .count(1'b1), .Q(counter_1_q), .carry(counter_1_carry), .clk(clock_1_out));  // open: load, D, clr
  Clock clock_1 (.out(clock_1_out));
  RGB_OUT rgb_out_1 (
    .PCLK(clock_1_out), .R(rgb_out_1_r), .out_14(rgb_out_1_out_14), .out_15(rgb_out_1_out_15),
    .out_16(rgb_out_1_out_16), .out_17(rgb_out_1_out_17), .out_18(rgb_out_1_out_18),
    .out_19(rgb_out_1_out_19), .out_20(rgb_out_1_out_20), .G(rgb_out_1_g), .out_22(rgb_out_1_out_22),
    .out_23(rgb_out_1_out_23), .out_24(rgb_out_1_out_24), .out_25(rgb_out_1_out_25),
    .out_26(rgb_out_1_out_26), .out_27(rgb_out_1_out_27), .out_28(rgb_out_1_out_28), .B(rgb_out_1_b),
    .out_30(rgb_out_1_out_30), .out_31(rgb_out_1_out_31), .out_32(rgb_out_1_out_32),
    .out_33(rgb_out_1_out_33), .out_34(rgb_out_1_out_34), .out_35(rgb_out_1_out_35),
    .out_36(rgb_out_1_out_36), .SYNC_2(rgb_out_1_sync_2), .PICTURE(1'b0), .nTR(1'b1), .nTG(1'b1), .nTB(1'b1),
    .nCC0(counter_1_q[2]), .nCC1(counter_1_q[3]), .nCC2(counter_1_q[4]), .nCC3(counter_1_q[5]),
    .SYNC(counter_1_carry), .nLL0(counter_1_q[0]), .nLL1(counter_1_q[1]));
endmodule

module D_LATCH (
  input  EN,
  input  D,
  output Q,
  output nQ
);

  D_Flip_Flop d_ff_1 (.clk(EN), .D(D), .Q(Q), .Qn(nQ));  // open: preset, en, reset
endmodule

// RGB OUT
module RGB_OUT (
  input  PCLK,
  input  PICTURE,
  input  nTR,
  input  nTG,
  input  nTB,
  input  nCC0,
  input  nCC1,
  input  nCC2,
  input  nCC3,
  input  nLL0,
  input  nLL1,
  input  SYNC,
  output R,
  output out_14,
  output out_15,
  output out_16,
  output out_17,
  output out_18,
  output out_19,
  output out_20,
  output G,
  output out_22,
  output out_23,
  output out_24,
  output out_25,
  output out_26,
  output out_27,
  output out_28,
  output B,
  output out_30,
  output out_31,
  output out_32,
  output out_33,
  output out_34,
  output out_35,
  output out_36,
  output SYNC_2
);

  wire and_1_out, and_2_out, and_3_out, and_4_out, and_5_out, and_6_out, and_7_out, and_8_out, and_9_out,
       d_latch_1_nq, d_latch_2_nq, d_latch_3_nq, d_latch_4_nq, d_latch_5_nq, d_latch_6_nq, d_latch_7_nq,
       d_latch_8_nq, d_latch_9_nq, d_latch_10_nq, d_latch_11_nq, d_latch_12_nq, d_latch_13_nq, d_latch_14_nq,
       d_latch_15_nq, nand_1_out, nand_2_out, nand_3_out, nand_4_out, nand_5_out, nand_6_out, nand_7_out,
       nand_8_out, nand_9_out, nor_1_out, nor_2_out, nor_3_out, nor_4_out, nor_5_out, nor_6_out, nor_7_out,
       nor_8_out, nor_9_out, nor_10_out, nor_11_out, nor_12_out, nor_13_out, nor_14_out, nor_15_out,
       nor_16_out, nor_17_out, nor_18_out, nor_19_out, nor_20_out, nor_21_out, nor_22_out, nor_23_out,
       nor_24_out, nor_25_out, nor_26_out, nor_27_out, nor_28_out, not_1_out, not_2_out, not_3_out,
       not_4_out, not_5_out, not_6_out, not_7_out, not_8_out, not_9_out, not_10_out, not_11_out, not_12_out,
       not_13_out, not_14_out, not_15_out, not_16_out, not_17_out, not_18_out, not_19_out, not_20_out,
       not_21_out, sel4x16_1__0, sel4x16_1__1, sel4x16_1__2, sel4x16_1__3, sel4x16_1__4, sel4x16_1__5,
       sel4x16_1__6, sel4x16_1__7, sel4x16_1__8, sel4x16_1__9, sel4x16_1__10, sel4x16_1__11, sel4x16_1__12,
       sel4x16_1__13, sel4x16_1__14, sel4x16_1__15, sel_12x3_1_out_17, sel_12x3_1_out_18, sel_12x3_1_out_19,
       sel_12x3_2_out_17, sel_12x3_2_out_18, sel_12x3_2_out_19, sel_12x3_3_out_17, sel_12x3_3_out_18,
       sel_12x3_3_out_19, sel_16x12_b_1_out_18, sel_16x12_b_1_out_19, sel_16x12_b_1_out_20,
       sel_16x12_b_1_out_21, sel_16x12_b_1_out_22, sel_16x12_b_1_out_23, sel_16x12_b_1_out_24,
       sel_16x12_b_1_out_25, sel_16x12_b_1_out_26, sel_16x12_b_1_out_27, sel_16x12_b_1_out_28,
       sel_16x12_b_1_out_29, sel_16x12_g_1_out_18, sel_16x12_g_1_out_19, sel_16x12_g_1_out_20,
       sel_16x12_g_1_out_21, sel_16x12_g_1_out_22, sel_16x12_g_1_out_23, sel_16x12_g_1_out_24,
       sel_16x12_g_1_out_25, sel_16x12_g_1_out_26, sel_16x12_g_1_out_27, sel_16x12_g_1_out_28,
       sel_16x12_g_1_out_29, sel_16x12_r_1_out_18, sel_16x12_r_1_out_19, sel_16x12_r_1_out_20,
       sel_16x12_r_1_out_21, sel_16x12_r_1_out_22, sel_16x12_r_1_out_23, sel_16x12_r_1_out_24,
       sel_16x12_r_1_out_25, sel_16x12_r_1_out_26, sel_16x12_r_1_out_27, sel_16x12_r_1_out_28,
       sel_16x12_r_1_out_29;

  D_LATCH d_latch_1 (.EN(not_1_out), .D(SYNC), .nQ(d_latch_1_nq));  // open: Q
  not not_1 (not_1_out, PCLK);
  D_LATCH d_latch_2 (.EN(PCLK), .D(nCC0), .nQ(d_latch_2_nq));  // open: Q
  D_LATCH d_latch_3 (.EN(PCLK), .D(nCC1), .nQ(d_latch_3_nq));  // open: Q
  D_LATCH d_latch_4 (.EN(PCLK), .D(nCC2), .nQ(d_latch_4_nq));  // open: Q
  D_LATCH d_latch_5 (.EN(PCLK), .D(nCC3), .nQ(d_latch_5_nq));  // open: Q
  D_LATCH d_latch_6 (.EN(PCLK), .D(nLL0), .nQ(d_latch_6_nq));  // open: Q
  D_LATCH d_latch_7 (.EN(PCLK), .D(nLL1), .nQ(d_latch_7_nq));  // open: Q
  D_LATCH d_latch_8 (.EN(PCLK), .D(d_latch_1_nq), .nQ(d_latch_8_nq));  // open: Q
  D_LATCH d_latch_9 (.EN(not_1_out), .D(d_latch_2_nq), .nQ(d_latch_9_nq));  // open: Q
  D_LATCH d_latch_10 (.EN(not_1_out), .D(d_latch_3_nq), .nQ(d_latch_10_nq));  // open: Q
  D_LATCH d_latch_11 (.EN(not_1_out), .D(d_latch_4_nq), .nQ(d_latch_11_nq));  // open: Q
  D_LATCH d_latch_12 (.EN(not_1_out), .D(d_latch_5_nq), .nQ(d_latch_12_nq));  // open: Q
  D_LATCH d_latch_13 (.EN(not_1_out), .D(d_latch_6_nq), .nQ(d_latch_13_nq));  // open: Q
  D_LATCH d_latch_14 (.EN(not_1_out), .D(d_latch_7_nq), .nQ(d_latch_14_nq));  // open: Q
  D_LATCH d_latch_15 (.EN(not_1_out), .D(d_latch_8_nq), .nQ(d_latch_15_nq));  // open: Q
  SEL4x16 sel4x16_1 (
    ._15(sel4x16_1__15), ._14(sel4x16_1__14), ._13(sel4x16_1__13), ._12(sel4x16_1__12), ._11(sel4x16_1__11),
    ._10(sel4x16_1__10), ._9(sel4x16_1__9), ._8(sel4x16_1__8), ._7(sel4x16_1__7), ._6(sel4x16_1__6),
    ._5(sel4x16_1__5), ._4(sel4x16_1__4), .C2(d_latch_11_nq), .C3(d_latch_12_nq), .L0(d_latch_13_nq),
    .L1(d_latch_14_nq), ._3(sel4x16_1__3), ._2(sel4x16_1__2), ._1(sel4x16_1__1), ._0(sel4x16_1__0),
    .PCLK(PCLK));
  SEL_16x12_R sel_16x12_r_1 (
    .out_18(sel_16x12_r_1_out_18), .out_19(sel_16x12_r_1_out_19), .out_20(sel_16x12_r_1_out_20),
    .out_21(sel_16x12_r_1_out_21), .out_22(sel_16x12_r_1_out_22), .out_23(sel_16x12_r_1_out_23),
    .out_24(sel_16x12_r_1_out_24), .out_25(sel_16x12_r_1_out_25), .out_26(sel_16x12_r_1_out_26),
    .out_27(sel_16x12_r_1_out_27), .out_28(sel_16x12_r_1_out_28), .out_29(sel_16x12_r_1_out_29),
    .in_2(sel4x16_1__15), .in_3(sel4x16_1__14), .in_4(sel4x16_1__13), .in_5(sel4x16_1__12),
    .in_6(sel4x16_1__11), .in_7(sel4x16_1__10), .in_8(sel4x16_1__9), .in_9(sel4x16_1__8),
    .in_10(sel4x16_1__7), .in_11(sel4x16_1__6), .in_12(sel4x16_1__5), .in_13(sel4x16_1__4),
    .in_14(sel4x16_1__3), .in_15(sel4x16_1__2), .in_16(sel4x16_1__1), .in_17(sel4x16_1__0), .PCLK(PCLK));
  SEL_16x12_G sel_16x12_g_1 (
    .out_18(sel_16x12_g_1_out_18), .out_19(sel_16x12_g_1_out_19), .out_20(sel_16x12_g_1_out_20),
    .out_21(sel_16x12_g_1_out_21), .out_22(sel_16x12_g_1_out_22), .out_23(sel_16x12_g_1_out_23),
    .out_24(sel_16x12_g_1_out_24), .out_25(sel_16x12_g_1_out_25), .out_26(sel_16x12_g_1_out_26),
    .out_27(sel_16x12_g_1_out_27), .out_28(sel_16x12_g_1_out_28), .out_29(sel_16x12_g_1_out_29),
    .in_2(sel4x16_1__15), .in_3(sel4x16_1__14), .in_4(sel4x16_1__13), .in_5(sel4x16_1__12),
    .in_6(sel4x16_1__11), .in_7(sel4x16_1__10), .in_8(sel4x16_1__9), .in_9(sel4x16_1__8),
    .in_10(sel4x16_1__7), .in_11(sel4x16_1__6), .in_12(sel4x16_1__5), .in_13(sel4x16_1__4),
    .in_14(sel4x16_1__3), .in_15(sel4x16_1__2), .in_16(sel4x16_1__1), .in_17(sel4x16_1__0), .PCLK(PCLK));
  SEL_16x12_B sel_16x12_b_1 (
    .out_18(sel_16x12_b_1_out_18), .out_19(sel_16x12_b_1_out_19), .out_20(sel_16x12_b_1_out_20),
    .out_21(sel_16x12_b_1_out_21), .out_22(sel_16x12_b_1_out_22), .out_23(sel_16x12_b_1_out_23),
    .out_24(sel_16x12_b_1_out_24), .out_25(sel_16x12_b_1_out_25), .out_26(sel_16x12_b_1_out_26),
    .out_27(sel_16x12_b_1_out_27), .out_28(sel_16x12_b_1_out_28), .out_29(sel_16x12_b_1_out_29),
    .in_2(sel4x16_1__15), .in_3(sel4x16_1__14), .in_4(sel4x16_1__13), .in_5(sel4x16_1__12),
    .in_6(sel4x16_1__11), .in_7(sel4x16_1__10), .in_8(sel4x16_1__9), .in_9(sel4x16_1__8),
    .in_10(sel4x16_1__7), .in_11(sel4x16_1__6), .in_12(sel4x16_1__5), .in_13(sel4x16_1__4),
    .in_14(sel4x16_1__3), .in_15(sel4x16_1__2), .in_16(sel4x16_1__1), .in_17(sel4x16_1__0), .PCLK(PCLK));
  nor nor_1 (nor_1_out, PCLK, d_latch_10_nq, not_2_out);
  not not_2 (not_2_out, d_latch_9_nq);
  not not_3 (not_3_out, d_latch_10_nq);
  SEL_12x3 sel_12x3_1 (
    .in_1(sel_16x12_r_1_out_18), .in_2(sel_16x12_r_1_out_19), .in_3(sel_16x12_r_1_out_20),
    .in_4(sel_16x12_r_1_out_21), .in_5(sel_16x12_r_1_out_22), .in_6(sel_16x12_r_1_out_23),
    .in_7(sel_16x12_r_1_out_24), .in_8(sel_16x12_r_1_out_25), .in_9(sel_16x12_r_1_out_26),
    .in_10(sel_16x12_r_1_out_27), .in_11(sel_16x12_r_1_out_28), .in_12(sel_16x12_r_1_out_29),
    .out_17(sel_12x3_1_out_17), .out_18(sel_12x3_1_out_18), .out_19(sel_12x3_1_out_19), ._1(nor_1_out),
    ._2(nor_3_out), ._3(nor_2_out), ._4(nor_4_out));
  SEL_12x3 sel_12x3_2 (
    .in_1(sel_16x12_g_1_out_18), .in_2(sel_16x12_g_1_out_19), .in_3(sel_16x12_g_1_out_20),
    .in_4(sel_16x12_g_1_out_21), .in_5(sel_16x12_g_1_out_22), .in_6(sel_16x12_g_1_out_23),
    .in_7(sel_16x12_g_1_out_24), .in_8(sel_16x12_g_1_out_25), .in_9(sel_16x12_g_1_out_26),
    .in_10(sel_16x12_g_1_out_27), .in_11(sel_16x12_g_1_out_28), .in_12(sel_16x12_g_1_out_29),
    .out_17(sel_12x3_2_out_17), .out_18(sel_12x3_2_out_18), .out_19(sel_12x3_2_out_19), ._1(nor_1_out),
    ._2(nor_3_out), ._3(nor_2_out), ._4(nor_4_out));
  SEL_12x3 sel_12x3_3 (
    .in_1(sel_16x12_b_1_out_18), .in_2(sel_16x12_b_1_out_19), .in_3(sel_16x12_b_1_out_20),
    .in_4(sel_16x12_b_1_out_21), .in_5(sel_16x12_b_1_out_22), .in_6(sel_16x12_b_1_out_23),
    .in_7(sel_16x12_b_1_out_24), .in_8(sel_16x12_b_1_out_25), .in_9(sel_16x12_b_1_out_26),
    .in_10(sel_16x12_b_1_out_27), .in_11(sel_16x12_b_1_out_28), .in_12(sel_16x12_b_1_out_29),
    .out_17(sel_12x3_3_out_17), .out_18(sel_12x3_3_out_18), .out_19(sel_12x3_3_out_19), ._1(nor_1_out),
    ._2(nor_3_out), ._3(nor_2_out), ._4(nor_4_out));
  nor nor_2 (nor_2_out, PCLK, not_3_out, not_2_out);
  nor nor_3 (nor_3_out, PCLK, d_latch_10_nq, d_latch_9_nq);
  not not_4 (not_4_out, sel_12x3_1_out_17);
  not not_5 (not_5_out, sel_12x3_1_out_18);
  not not_6 (not_6_out, sel_12x3_1_out_19);
  not not_7 (not_7_out, sel_12x3_2_out_17);
  not not_8 (not_8_out, sel_12x3_2_out_18);
  not not_9 (not_9_out, sel_12x3_2_out_19);
  not not_10 (not_10_out, sel_12x3_3_out_17);
  not not_11 (not_11_out, sel_12x3_3_out_18);
  not not_12 (not_12_out, sel_12x3_3_out_19);
  nor nor_4 (nor_4_out, PCLK, not_3_out, d_latch_9_nq);
  nand nand_1 (nand_1_out, nTR, not_4_out);
  nand nand_2 (nand_2_out, nTR, not_5_out);
  nand nand_3 (nand_3_out, nTR, not_6_out);
  nand nand_4 (nand_4_out, nTG, not_7_out);
  nand nand_5 (nand_5_out, nTG, not_8_out);
  nand nand_6 (nand_6_out, nTG, not_9_out);
  nand nand_7 (nand_7_out, nTB, not_10_out);
  nand nand_8 (nand_8_out, nTB, not_11_out);
  nand nand_9 (nand_9_out, nTB, not_12_out);
  and and_1 (and_1_out, ~PICTURE, nand_1_out);  // AND_Gate
  and and_2 (and_2_out, ~PICTURE, nand_2_out);  // AND_Gate
  and and_3 (and_3_out, ~PICTURE, nand_3_out);  // AND_Gate
  and and_4 (and_4_out, ~PICTURE, nand_4_out);  // AND_Gate
  and and_5 (and_5_out, ~PICTURE, nand_5_out);  // AND_Gate
  and and_6 (and_6_out, ~PICTURE, nand_6_out);  // AND_Gate
  and and_7 (and_7_out, ~PICTURE, nand_7_out);  // AND_Gate
  and and_8 (and_8_out, ~PICTURE, nand_8_out);  // AND_Gate
  and and_9 (and_9_out, ~PICTURE, nand_9_out);  // AND_Gate
  not not_13 (not_13_out, and_3_out);
  not not_14 (not_14_out, and_2_out);
  not not_15 (not_15_out, and_5_out);
  not not_16 (not_16_out, and_6_out);
  not not_17 (not_17_out, and_8_out);
  not not_18 (not_18_out, and_9_out);
  not not_19 (not_19_out, and_1_out);
  not not_20 (not_20_out, and_4_out);
  not not_21 (not_21_out, and_7_out);
  and and_10 (R, not_1_out, nor_5_out);
  nor nor_5 (nor_5_out, and_1_out, and_2_out, and_3_out);
  and and_11 (out_14, not_1_out, nor_6_out);
  nor nor_6 (nor_6_out, and_1_out, and_2_out, not_13_out);
  and and_12 (out_15, not_1_out, nor_7_out);
  nor nor_7 (nor_7_out, and_3_out, not_14_out, and_1_out);
  and and_13 (out_16, not_1_out, nor_8_out);
  nor nor_8 (nor_8_out, not_13_out, not_14_out, and_1_out);
  and and_14 (out_17, not_1_out, nor_9_out);
  nor nor_9 (nor_9_out, and_3_out, and_2_out, not_19_out);
  and and_15 (out_18, not_1_out, nor_10_out);
  nor nor_10 (nor_10_out, not_13_out, and_2_out, not_19_out);
  and and_16 (out_19, not_1_out, nor_11_out);
  nor nor_11 (nor_11_out, and_3_out, not_14_out, not_19_out);
  and and_17 (out_20, not_1_out, nor_12_out);
  nor nor_12 (nor_12_out, not_13_out, not_14_out, not_19_out);
  and and_18 (G, not_1_out, nor_13_out);
  nor nor_13 (nor_13_out, and_4_out, and_5_out, and_6_out);
  and and_19 (out_22, not_1_out, nor_14_out);
  nor nor_14 (nor_14_out, and_4_out, and_5_out, not_16_out);
  and and_20 (out_23, not_1_out, nor_15_out);
  nor nor_15 (nor_15_out, and_6_out, not_15_out, and_4_out);
  and and_21 (out_24, not_1_out, nor_16_out);
  nor nor_16 (nor_16_out, not_16_out, not_15_out, and_4_out);
  and and_22 (out_25, not_1_out, nor_17_out);
  nor nor_17 (nor_17_out, and_6_out, and_5_out, not_20_out);
  and and_23 (out_26, not_1_out, nor_18_out);
  nor nor_18 (nor_18_out, not_16_out, and_5_out, not_20_out);
  and and_24 (out_27, not_1_out, nor_19_out);
  nor nor_19 (nor_19_out, and_6_out, not_15_out, not_20_out);
  and and_25 (out_28, not_1_out, nor_20_out);
  nor nor_20 (nor_20_out, not_16_out, not_15_out, not_20_out);
  and and_26 (B, not_1_out, nor_21_out);
  nor nor_21 (nor_21_out, and_7_out, and_8_out, and_9_out);
  and and_27 (out_30, not_1_out, nor_22_out);
  nor nor_22 (nor_22_out, and_7_out, and_8_out, not_18_out);
  and and_28 (out_31, not_1_out, nor_23_out);
  nor nor_23 (nor_23_out, and_9_out, not_17_out, and_7_out);
  and and_29 (out_32, not_1_out, nor_24_out);
  nor nor_24 (nor_24_out, not_18_out, not_17_out, and_7_out);
  and and_30 (out_33, not_1_out, nor_25_out);
  nor nor_25 (nor_25_out, and_9_out, and_8_out, not_21_out);
  and and_31 (out_34, not_1_out, nor_26_out);
  nor nor_26 (nor_26_out, not_18_out, and_8_out, not_21_out);
  and and_32 (out_35, not_1_out, nor_27_out);
  nor nor_27 (nor_27_out, and_9_out, not_17_out, not_21_out);
  and and_33 (out_36, not_1_out, nor_28_out);
  nor nor_28 (nor_28_out, not_18_out, not_17_out, not_21_out);
  not not_22 (SYNC_2, d_latch_15_nq);

  // Notes on the sheet:
  //   2
  //   1
  //   0
  //   2
  //   1
  //   0
  //   2
  //   1
  //   0
endmodule

module SEL_12x3 (
  input  in_1,
  input  in_2,
  input  in_3,
  input  in_4,
  input  in_5,
  input  in_6,
  input  in_7,
  input  in_8,
  input  in_9,
  input  in_10,
  input  in_11,
  input  in_12,
  input  _1,
  input  _2,
  input  _3,
  input  _4,
  output out_17,
  output out_18,
  output out_19
);

  wire and_1_out, and_2_out, and_3_out, and_4_out, and_5_out, and_6_out, and_7_out, and_8_out, and_9_out,
       and_10_out, and_11_out, and_12_out;

  and and_1 (and_1_out, in_1, _1);
  and and_2 (and_2_out, in_2, _2);
  and and_3 (and_3_out, in_3, _3);
  and and_4 (and_4_out, in_4, _4);
  and and_5 (and_5_out, in_5, _1);
  and and_6 (and_6_out, in_6, _2);
  and and_7 (and_7_out, in_7, _3);
  and and_8 (and_8_out, in_8, _4);
  and and_9 (and_9_out, in_9, _1);
  and and_10 (and_10_out, in_10, _2);
  and and_11 (and_11_out, in_11, _3);
  and and_12 (and_12_out, in_12, _4);
  or or_1 (out_17, and_1_out, and_2_out, and_3_out, and_4_out);
  or or_2 (out_18, and_5_out, and_6_out, and_7_out, and_8_out);
  or or_3 (out_19, and_9_out, and_10_out, and_11_out, and_12_out);
endmodule

module SEL_16x12_R (
  input  PCLK,
  input  in_2,
  input  in_3,
  input  in_4,
  input  in_5,
  input  in_6,
  input  in_7,
  input  in_8,
  input  in_9,
  input  in_10,
  input  in_11,
  input  in_12,
  input  in_13,
  input  in_14,
  input  in_15,
  input  in_16,
  input  in_17,
  output out_18,
  output out_19,
  output out_20,
  output out_21,
  output out_22,
  output out_23,
  output out_24,
  output out_25,
  output out_26,
  output out_27,
  output out_28,
  output out_29
);

  wire not_1_out, transistor_1_out, transistor_2_out, transistor_3_out, transistor_5_out, transistor_7_out,
       transistor_9_out, transistor_10_out, transistor_12_out, transistor_15_out, transistor_17_out,
       transistor_18_out, transistor_34_out;

  not not_1 (not_1_out, PCLK);
  and and_1 (out_18, not_1_out, transistor_1_out);
  and and_2 (out_19, not_1_out, transistor_12_out);
  and and_3 (out_20, not_1_out, transistor_34_out);
  and and_4 (out_21, not_1_out, transistor_2_out);
  and and_5 (out_22, not_1_out, transistor_3_out);
  and and_6 (out_23, not_1_out, transistor_15_out);
  and and_7 (out_24, not_1_out, transistor_5_out);
  and and_8 (out_25, not_1_out, transistor_7_out);
  and and_9 (out_26, not_1_out, transistor_17_out);
  and and_10 (out_27, not_1_out, transistor_18_out);
  and and_11 (out_28, not_1_out, transistor_9_out);
  and and_12 (out_29, not_1_out, transistor_10_out);
  Transistor #(.\type ("n")) transistor_1 (.in(1'b0), .out(transistor_1_out), .gate(in_3));
  Transistor #(.\type ("n")) transistor_2 (.in(1'b0), .out(transistor_2_out), .gate(in_3));
  Transistor #(.\type ("n")) transistor_3 (.in(1'b0), .out(transistor_3_out), .gate(in_2));
  Transistor #(.\type ("n")) transistor_4 (.in(1'b0), .out(transistor_3_out), .gate(in_3));
  Transistor #(.\type ("n")) transistor_5 (.in(1'b0), .out(transistor_5_out), .gate(in_3));
  Transistor #(.\type ("n")) transistor_6 (.in(1'b0), .out(transistor_5_out), .gate(in_2));
  Transistor #(.\type ("n")) transistor_7 (.in(1'b0), .out(transistor_7_out), .gate(in_3));
  Transistor #(.\type ("n")) transistor_8 (.in(1'b0), .out(transistor_7_out), .gate(in_2));
  Transistor #(.\type ("n")) transistor_9 (.in(1'b0), .out(transistor_9_out), .gate(in_2));
  Transistor #(.\type ("n")) transistor_10 (.in(1'b0), .out(transistor_10_out), .gate(in_3));
  Transistor #(.\type ("n")) transistor_11 (.in(1'b0), .out(transistor_1_out), .gate(in_4));
  Transistor #(.\type ("n")) transistor_12 (.in(1'b0), .out(transistor_12_out), .gate(in_4));
  Transistor #(.\type ("n")) transistor_13 (.in(1'b0), .out(transistor_2_out), .gate(in_4));
  Transistor #(.\type ("n")) transistor_14 (.in(1'b0), .out(transistor_3_out), .gate(in_5));
  Transistor #(.\type ("n")) transistor_15 (.in(1'b0), .out(transistor_15_out), .gate(in_4));
  Transistor #(.\type ("n")) transistor_16 (.in(1'b0), .out(transistor_7_out), .gate(in_4));
  Transistor #(.\type ("n")) transistor_17 (.in(1'b0), .out(transistor_17_out), .gate(in_5));
  Transistor #(.\type ("n")) transistor_18 (.in(1'b0), .out(transistor_18_out), .gate(in_5));
  Transistor #(.\type ("n")) transistor_19 (.in(1'b0), .out(transistor_18_out), .gate(in_4));
  Transistor #(.\type ("n")) transistor_20 (.in(1'b0), .out(transistor_9_out), .gate(in_5));
  Transistor #(.\type ("n")) transistor_21 (.in(1'b0), .out(transistor_10_out), .gate(in_4));
  Transistor #(.\type ("n")) transistor_22 (.in(1'b0), .out(transistor_1_out), .gate(in_6));
  Transistor #(.\type ("n")) transistor_23 (.in(1'b0), .out(transistor_12_out), .gate(in_6));
  Transistor #(.\type ("n")) transistor_24 (.in(1'b0), .out(transistor_3_out), .gate(in_6));
  Transistor #(.\type ("n")) transistor_25 (.in(1'b0), .out(transistor_15_out), .gate(in_6));
  Transistor #(.\type ("n")) transistor_26 (.in(1'b0), .out(transistor_5_out), .gate(in_6));
  Transistor #(.\type ("n")) transistor_27 (.in(1'b0), .out(transistor_7_out), .gate(in_6));
  Transistor #(.\type ("n")) transistor_28 (.in(1'b0), .out(transistor_17_out), .gate(in_6));
  Transistor #(.\type ("n")) transistor_29 (.in(1'b0), .out(transistor_18_out), .gate(in_6));
  Transistor #(.\type ("n")) transistor_30 (.in(1'b0), .out(transistor_10_out), .gate(in_6));
  Transistor #(.\type ("n")) transistor_31 (.in(1'b0), .out(transistor_1_out), .gate(in_8));
  Transistor #(.\type ("n")) transistor_32 (.in(1'b0), .out(transistor_1_out), .gate(in_7));
  Transistor #(.\type ("n")) transistor_33 (.in(1'b0), .out(transistor_12_out), .gate(in_8));
  Transistor #(.\type ("n")) transistor_34 (.in(1'b0), .out(transistor_34_out), .gate(in_8));
  Transistor #(.\type ("n")) transistor_35 (.in(1'b0), .out(transistor_2_out), .gate(in_7));
  Transistor #(.\type ("n")) transistor_36 (.in(1'b0), .out(transistor_2_out), .gate(in_8));
  Transistor #(.\type ("n")) transistor_37 (.in(1'b0), .out(transistor_3_out), .gate(in_7));
  Transistor #(.\type ("n")) transistor_38 (.in(1'b0), .out(transistor_3_out), .gate(in_8));
  Transistor #(.\type ("n")) transistor_39 (.in(1'b0), .out(transistor_15_out), .gate(in_7));
  Transistor #(.\type ("n")) transistor_40 (.in(1'b0), .out(transistor_5_out), .gate(in_8));
  Transistor #(.\type ("n")) transistor_41 (.in(1'b0), .out(transistor_7_out), .gate(in_7));
  Transistor #(.\type ("n")) transistor_42 (.in(1'b0), .out(transistor_17_out), .gate(in_7));
  Transistor #(.\type ("n")) transistor_43 (.in(1'b0), .out(transistor_17_out), .gate(in_8));
  Transistor #(.\type ("n")) transistor_44 (.in(1'b0), .out(transistor_18_out), .gate(in_7));
  Transistor #(.\type ("n")) transistor_45 (.in(1'b0), .out(transistor_9_out), .gate(in_8));
  Transistor #(.\type ("n")) transistor_46 (.in(1'b0), .out(transistor_9_out), .gate(in_7));
  Transistor #(.\type ("n")) transistor_47 (.in(1'b0), .out(transistor_15_out), .gate(in_9));
  Transistor #(.\type ("n")) transistor_48 (.in(1'b0), .out(transistor_12_out), .gate(in_10));
  Transistor #(.\type ("n")) transistor_49 (.in(1'b0), .out(transistor_34_out), .gate(in_10));
  Transistor #(.\type ("n")) transistor_50 (.in(1'b0), .out(transistor_2_out), .gate(in_11));
  Transistor #(.\type ("n")) transistor_51 (.in(1'b0), .out(transistor_15_out), .gate(in_10));
  Transistor #(.\type ("n")) transistor_52 (.in(1'b0), .out(transistor_5_out), .gate(in_10));
  Transistor #(.\type ("n")) transistor_53 (.in(1'b0), .out(transistor_7_out), .gate(in_11));
  Transistor #(.\type ("n")) transistor_54 (.in(1'b0), .out(transistor_18_out), .gate(in_10));
  Transistor #(.\type ("n")) transistor_55 (.in(1'b0), .out(transistor_9_out), .gate(in_10));
  Transistor #(.\type ("n")) transistor_56 (.in(1'b0), .out(transistor_10_out), .gate(in_10));
  Transistor #(.\type ("n")) transistor_57 (.in(1'b0), .out(transistor_1_out), .gate(in_13));
  Transistor #(.\type ("n")) transistor_58 (.in(1'b0), .out(transistor_34_out), .gate(in_12));
  Transistor #(.\type ("n")) transistor_59 (.in(1'b0), .out(transistor_34_out), .gate(in_13));
  Transistor #(.\type ("n")) transistor_60 (.in(1'b0), .out(transistor_2_out), .gate(in_12));
  Transistor #(.\type ("n")) transistor_61 (.in(1'b0), .out(transistor_2_out), .gate(in_13));
  Transistor #(.\type ("n")) transistor_62 (.in(1'b0), .out(transistor_15_out), .gate(in_12));
  Transistor #(.\type ("n")) transistor_63 (.in(1'b0), .out(transistor_15_out), .gate(in_13));
  Transistor #(.\type ("n")) transistor_64 (.in(1'b0), .out(transistor_5_out), .gate(in_13));
  Transistor #(.\type ("n")) transistor_65 (.in(1'b0), .out(transistor_7_out), .gate(in_13));
  Transistor #(.\type ("n")) transistor_66 (.in(1'b0), .out(transistor_18_out), .gate(in_12));
  Transistor #(.\type ("n")) transistor_67 (.in(1'b0), .out(transistor_18_out), .gate(in_13));
  Transistor #(.\type ("n")) transistor_68 (.in(1'b0), .out(transistor_9_out), .gate(in_13));
  Transistor #(.\type ("n")) transistor_69 (.in(1'b0), .out(transistor_10_out), .gate(in_13));
  Transistor #(.\type ("n")) transistor_70 (.in(1'b0), .out(transistor_12_out), .gate(in_14));
  Transistor #(.\type ("n")) transistor_71 (.in(1'b0), .out(transistor_2_out), .gate(in_14));
  Transistor #(.\type ("n")) transistor_72 (.in(1'b0), .out(transistor_5_out), .gate(in_14));
  Transistor #(.\type ("n")) transistor_73 (.in(1'b0), .out(transistor_7_out), .gate(in_14));
  Transistor #(.\type ("n")) transistor_74 (.in(1'b0), .out(transistor_18_out), .gate(in_14));
  Transistor #(.\type ("n")) transistor_75 (.in(1'b0), .out(transistor_10_out), .gate(in_14));
  Transistor #(.\type ("n")) transistor_76 (.in(1'b0), .out(transistor_1_out), .gate(in_15));
  Transistor #(.\type ("n")) transistor_77 (.in(1'b0), .out(transistor_12_out), .gate(in_15));
  Transistor #(.\type ("n")) transistor_78 (.in(1'b0), .out(transistor_12_out), .gate(in_16));
  Transistor #(.\type ("n")) transistor_79 (.in(1'b0), .out(transistor_2_out), .gate(in_16));
  Transistor #(.\type ("n")) transistor_80 (.in(1'b0), .out(transistor_15_out), .gate(in_16));
  Transistor #(.\type ("n")) transistor_81 (.in(1'b0), .out(transistor_15_out), .gate(in_15));
  Transistor #(.\type ("n")) transistor_82 (.in(1'b0), .out(transistor_7_out), .gate(in_16));
  Transistor #(.\type ("n")) transistor_83 (.in(1'b0), .out(transistor_7_out), .gate(in_15));
  Transistor #(.\type ("n")) transistor_84 (.in(1'b0), .out(transistor_17_out), .gate(in_15));
  Transistor #(.\type ("n")) transistor_85 (.in(1'b0), .out(transistor_18_out), .gate(in_15));
  Transistor #(.\type ("n")) transistor_86 (.in(1'b0), .out(transistor_18_out), .gate(in_16));
  Transistor #(.\type ("n")) transistor_87 (.in(1'b0), .out(transistor_9_out), .gate(in_15));
  Transistor #(.\type ("n")) transistor_88 (.in(1'b0), .out(transistor_9_out), .gate(in_16));
  Transistor #(.\type ("n")) transistor_89 (.in(1'b0), .out(transistor_10_out), .gate(in_16));
  Transistor #(.\type ("n")) transistor_90 (.in(1'b0), .out(transistor_10_out), .gate(in_15));
  Transistor #(.\type ("n")) transistor_91 (.in(1'b0), .out(transistor_1_out), .gate(in_17));
  Transistor #(.\type ("n")) transistor_92 (.in(1'b0), .out(transistor_12_out), .gate(in_17));
  Transistor #(.\type ("n")) transistor_93 (.in(1'b0), .out(transistor_3_out), .gate(in_17));
  Transistor #(.\type ("n")) transistor_94 (.in(1'b0), .out(transistor_7_out), .gate(in_17));
  Transistor #(.\type ("n")) transistor_95 (.in(1'b0), .out(transistor_17_out), .gate(in_17));
  Transistor #(.\type ("n")) transistor_96 (.in(1'b0), .out(transistor_18_out), .gate(in_17));
  Transistor #(.\type ("n")) transistor_97 (.in(1'b0), .out(transistor_10_out), .gate(in_17));
  Pull_Resistor #(.pull(1)) pull_resistor_1 (.node(transistor_1_out));
  Pull_Resistor #(.pull(1)) pull_resistor_2 (.node(transistor_12_out));
  Pull_Resistor #(.pull(1)) pull_resistor_3 (.node(transistor_34_out));
  Pull_Resistor #(.pull(1)) pull_resistor_4 (.node(transistor_2_out));
  Pull_Resistor #(.pull(1)) pull_resistor_5 (.node(transistor_3_out));
  Pull_Resistor #(.pull(1)) pull_resistor_6 (.node(transistor_15_out));
  Pull_Resistor #(.pull(1)) pull_resistor_7 (.node(transistor_5_out));
  Pull_Resistor #(.pull(1)) pull_resistor_8 (.node(transistor_7_out));
  Pull_Resistor #(.pull(1)) pull_resistor_9 (.node(transistor_17_out));
  Pull_Resistor #(.pull(1)) pull_resistor_10 (.node(transistor_18_out));
  Pull_Resistor #(.pull(1)) pull_resistor_11 (.node(transistor_9_out));
  Pull_Resistor #(.pull(1)) pull_resistor_12 (.node(transistor_10_out));
endmodule

module SEL_16x12_G (
  input  PCLK,
  input  in_2,
  input  in_3,
  input  in_4,
  input  in_5,
  input  in_6,
  input  in_7,
  input  in_8,
  input  in_9,
  input  in_10,
  input  in_11,
  input  in_12,
  input  in_13,
  input  in_14,
  input  in_15,
  input  in_16,
  input  in_17,
  output out_18,
  output out_19,
  output out_20,
  output out_21,
  output out_22,
  output out_23,
  output out_24,
  output out_25,
  output out_26,
  output out_27,
  output out_28,
  output out_29
);

  wire not_1_out, transistor_1_out, transistor_2_out, transistor_3_out, transistor_4_out, transistor_5_out,
       transistor_7_out, transistor_8_out, transistor_9_out, transistor_15_out, transistor_16_out,
       transistor_21_out, transistor_26_out;

  not not_1 (not_1_out, PCLK);
  and and_1 (out_18, not_1_out, transistor_1_out);
  and and_2 (out_19, not_1_out, transistor_2_out);
  and and_3 (out_20, not_1_out, transistor_26_out);
  and and_4 (out_21, not_1_out, transistor_3_out);
  and and_5 (out_22, not_1_out, transistor_4_out);
  and and_6 (out_23, not_1_out, transistor_15_out);
  and and_7 (out_24, not_1_out, transistor_16_out);
  and and_8 (out_25, not_1_out, transistor_5_out);
  and and_9 (out_26, not_1_out, transistor_7_out);
  and and_10 (out_27, not_1_out, transistor_21_out);
  and and_11 (out_28, not_1_out, transistor_8_out);
  and and_12 (out_29, not_1_out, transistor_9_out);
  Transistor #(.\type ("n")) transistor_1 (.in(1'b0), .out(transistor_1_out), .gate(in_3));
  Transistor #(.\type ("n")) transistor_2 (.in(1'b0), .out(transistor_2_out), .gate(in_2));
  Transistor #(.\type ("n")) transistor_3 (.in(1'b0), .out(transistor_3_out), .gate(in_2));
  Transistor #(.\type ("n")) transistor_4 (.in(1'b0), .out(transistor_4_out), .gate(in_2));
  Transistor #(.\type ("n")) transistor_5 (.in(1'b0), .out(transistor_5_out), .gate(in_3));
  Transistor #(.\type ("n")) transistor_6 (.in(1'b0), .out(transistor_5_out), .gate(in_2));
  Transistor #(.\type ("n")) transistor_7 (.in(1'b0), .out(transistor_7_out), .gate(in_3));
  Transistor #(.\type ("n")) transistor_8 (.in(1'b0), .out(transistor_8_out), .gate(in_3));
  Transistor #(.\type ("n")) transistor_9 (.in(1'b0), .out(transistor_9_out), .gate(in_3));
  Transistor #(.\type ("n")) transistor_10 (.in(1'b0), .out(transistor_9_out), .gate(in_2));
  Transistor #(.\type ("n")) transistor_11 (.in(1'b0), .out(transistor_1_out), .gate(in_4));
  Transistor #(.\type ("n")) transistor_12 (.in(1'b0), .out(transistor_2_out), .gate(in_4));
  Transistor #(.\type ("n")) transistor_13 (.in(1'b0), .out(transistor_3_out), .gate(in_4));
  Transistor #(.\type ("n")) transistor_14 (.in(1'b0), .out(transistor_3_out), .gate(in_5));
  Transistor #(.\type ("n")) transistor_15 (.in(1'b0), .out(transistor_15_out), .gate(in_4));
  Transistor #(.\type ("n")) transistor_16 (.in(1'b0), .out(transistor_16_out), .gate(in_5));
  Transistor #(.\type ("n")) transistor_17 (.in(1'b0), .out(transistor_5_out), .gate(in_5));
  Transistor #(.\type ("n")) transistor_18 (.in(1'b0), .out(transistor_5_out), .gate(in_4));
  Transistor #(.\type ("n")) transistor_19 (.in(1'b0), .out(transistor_7_out), .gate(in_5));
  Transistor #(.\type ("n")) transistor_20 (.in(1'b0), .out(transistor_7_out), .gate(in_4));
  Transistor #(.\type ("n")) transistor_21 (.in(1'b0), .out(transistor_21_out), .gate(in_4));
  Transistor #(.\type ("n")) transistor_22 (.in(1'b0), .out(transistor_21_out), .gate(in_5));
  Transistor #(.\type ("n")) transistor_23 (.in(1'b0), .out(transistor_8_out), .gate(in_4));
  Transistor #(.\type ("n")) transistor_24 (.in(1'b0), .out(transistor_9_out), .gate(in_5));
  Transistor #(.\type ("n")) transistor_25 (.in(1'b0), .out(transistor_1_out), .gate(in_6));
  Transistor #(.\type ("n")) transistor_26 (.in(1'b0), .out(transistor_26_out), .gate(in_6));
  Transistor #(.\type ("n")) transistor_27 (.in(1'b0), .out(transistor_15_out), .gate(in_6));
  Transistor #(.\type ("n")) transistor_28 (.in(1'b0), .out(transistor_16_out), .gate(in_6));
  Transistor #(.\type ("n")) transistor_29 (.in(1'b0), .out(transistor_5_out), .gate(in_6));
  Transistor #(.\type ("n")) transistor_30 (.in(1'b0), .out(transistor_7_out), .gate(in_6));
  Transistor #(.\type ("n")) transistor_31 (.in(1'b0), .out(transistor_21_out), .gate(in_6));
  Transistor #(.\type ("n")) transistor_32 (.in(1'b0), .out(transistor_8_out), .gate(in_6));
  Transistor #(.\type ("n")) transistor_33 (.in(1'b0), .out(transistor_9_out), .gate(in_6));
  Transistor #(.\type ("n")) transistor_34 (.in(1'b0), .out(transistor_1_out), .gate(in_8));
  Transistor #(.\type ("n")) transistor_35 (.in(1'b0), .out(transistor_2_out), .gate(in_8));
  Transistor #(.\type ("n")) transistor_36 (.in(1'b0), .out(transistor_2_out), .gate(in_7));
  Transistor #(.\type ("n")) transistor_37 (.in(1'b0), .out(transistor_26_out), .gate(in_8));
  Transistor #(.\type ("n")) transistor_38 (.in(1'b0), .out(transistor_26_out), .gate(in_7));
  Transistor #(.\type ("n")) transistor_39 (.in(1'b0), .out(transistor_3_out), .gate(in_8));
  Transistor #(.\type ("n")) transistor_40 (.in(1'b0), .out(transistor_4_out), .gate(in_7));
  Transistor #(.\type ("n")) transistor_41 (.in(1'b0), .out(transistor_4_out), .gate(in_8));
  Transistor #(.\type ("n")) transistor_42 (.in(1'b0), .out(transistor_16_out), .gate(in_8));
  Transistor #(.\type ("n")) transistor_43 (.in(1'b0), .out(transistor_5_out), .gate(in_7));
  Transistor #(.\type ("n")) transistor_44 (.in(1'b0), .out(transistor_7_out), .gate(in_8));
  Transistor #(.\type ("n")) transistor_45 (.in(1'b0), .out(transistor_21_out), .gate(in_8));
  Transistor #(.\type ("n")) transistor_46 (.in(1'b0), .out(transistor_8_out), .gate(in_8));
  Transistor #(.\type ("n")) transistor_47 (.in(1'b0), .out(transistor_9_out), .gate(in_7));
  Transistor #(.\type ("n")) transistor_48 (.in(1'b0), .out(transistor_2_out), .gate(in_9));
  Transistor #(.\type ("n")) transistor_49 (.in(1'b0), .out(transistor_3_out), .gate(in_9));
  Transistor #(.\type ("n")) transistor_50 (.in(1'b0), .out(transistor_4_out), .gate(in_9));
  Transistor #(.\type ("n")) transistor_51 (.in(1'b0), .out(transistor_15_out), .gate(in_9));
  Transistor #(.\type ("n")) transistor_52 (.in(1'b0), .out(transistor_16_out), .gate(in_9));
  Transistor #(.\type ("n")) transistor_53 (.in(1'b0), .out(transistor_5_out), .gate(in_9));
  Transistor #(.\type ("n")) transistor_54 (.in(1'b0), .out(transistor_8_out), .gate(in_9));
  Transistor #(.\type ("n")) transistor_55 (.in(1'b0), .out(transistor_9_out), .gate(in_9));
  Transistor #(.\type ("n")) transistor_56 (.in(1'b0), .out(transistor_2_out), .gate(in_10));
  Transistor #(.\type ("n")) transistor_57 (.in(1'b0), .out(transistor_26_out), .gate(in_10));
  Transistor #(.\type ("n")) transistor_58 (.in(1'b0), .out(transistor_3_out), .gate(in_10));
  Transistor #(.\type ("n")) transistor_59 (.in(1'b0), .out(transistor_3_out), .gate(in_11));
  Transistor #(.\type ("n")) transistor_60 (.in(1'b0), .out(transistor_15_out), .gate(in_11));
  Transistor #(.\type ("n")) transistor_61 (.in(1'b0), .out(transistor_16_out), .gate(in_11));
  Transistor #(.\type ("n")) transistor_62 (.in(1'b0), .out(transistor_16_out), .gate(in_10));
  Transistor #(.\type ("n")) transistor_63 (.in(1'b0), .out(transistor_5_out), .gate(in_11));
  Transistor #(.\type ("n")) transistor_64 (.in(1'b0), .out(transistor_21_out), .gate(in_10));
  Transistor #(.\type ("n")) transistor_65 (.in(1'b0), .out(transistor_8_out), .gate(in_11));
  Transistor #(.\type ("n")) transistor_66 (.in(1'b0), .out(transistor_8_out), .gate(in_10));
  Transistor #(.\type ("n")) transistor_67 (.in(1'b0), .out(transistor_1_out), .gate(in_13));
  Transistor #(.\type ("n")) transistor_68 (.in(1'b0), .out(transistor_1_out), .gate(in_12));
  Transistor #(.\type ("n")) transistor_69 (.in(1'b0), .out(transistor_2_out), .gate(in_12));
  Transistor #(.\type ("n")) transistor_70 (.in(1'b0), .out(transistor_26_out), .gate(in_13));
  Transistor #(.\type ("n")) transistor_71 (.in(1'b0), .out(transistor_3_out), .gate(in_13));
  Transistor #(.\type ("n")) transistor_72 (.in(1'b0), .out(transistor_4_out), .gate(in_12));
  Transistor #(.\type ("n")) transistor_73 (.in(1'b0), .out(transistor_4_out), .gate(in_13));
  Transistor #(.\type ("n")) transistor_74 (.in(1'b0), .out(transistor_15_out), .gate(in_13));
  Transistor #(.\type ("n")) transistor_75 (.in(1'b0), .out(transistor_15_out), .gate(in_12));
  Transistor #(.\type ("n")) transistor_76 (.in(1'b0), .out(transistor_16_out), .gate(in_13));
  Transistor #(.\type ("n")) transistor_77 (.in(1'b0), .out(transistor_16_out), .gate(in_12));
  Transistor #(.\type ("n")) transistor_78 (.in(1'b0), .out(transistor_7_out), .gate(in_12));
  Transistor #(.\type ("n")) transistor_79 (.in(1'b0), .out(transistor_21_out), .gate(in_13));
  Transistor #(.\type ("n")) transistor_80 (.in(1'b0), .out(transistor_21_out), .gate(in_12));
  Transistor #(.\type ("n")) transistor_81 (.in(1'b0), .out(transistor_8_out), .gate(in_13));
  Transistor #(.\type ("n")) transistor_82 (.in(1'b0), .out(transistor_9_out), .gate(in_12));
  Transistor #(.\type ("n")) transistor_83 (.in(1'b0), .out(transistor_2_out), .gate(in_14));
  Transistor #(.\type ("n")) transistor_84 (.in(1'b0), .out(transistor_4_out), .gate(in_14));
  Transistor #(.\type ("n")) transistor_85 (.in(1'b0), .out(transistor_15_out), .gate(in_14));
  Transistor #(.\type ("n")) transistor_86 (.in(1'b0), .out(transistor_21_out), .gate(in_14));
  Transistor #(.\type ("n")) transistor_87 (.in(1'b0), .out(transistor_1_out), .gate(in_15));
  Transistor #(.\type ("n")) transistor_88 (.in(1'b0), .out(transistor_2_out), .gate(in_16));
  Transistor #(.\type ("n")) transistor_89 (.in(1'b0), .out(transistor_3_out), .gate(in_16));
  Transistor #(.\type ("n")) transistor_90 (.in(1'b0), .out(transistor_3_out), .gate(in_15));
  Transistor #(.\type ("n")) transistor_91 (.in(1'b0), .out(transistor_4_out), .gate(in_16));
  Transistor #(.\type ("n")) transistor_92 (.in(1'b0), .out(transistor_15_out), .gate(in_16));
  Transistor #(.\type ("n")) transistor_93 (.in(1'b0), .out(transistor_16_out), .gate(in_16));
  Transistor #(.\type ("n")) transistor_94 (.in(1'b0), .out(transistor_7_out), .gate(in_15));
  Transistor #(.\type ("n")) transistor_95 (.in(1'b0), .out(transistor_21_out), .gate(in_16));
  Transistor #(.\type ("n")) transistor_96 (.in(1'b0), .out(transistor_8_out), .gate(in_15));
  Transistor #(.\type ("n")) transistor_97 (.in(1'b0), .out(transistor_9_out), .gate(in_15));
  Transistor #(.\type ("n")) transistor_98 (.in(1'b0), .out(transistor_1_out), .gate(in_17));
  Transistor #(.\type ("n")) transistor_99 (.in(1'b0), .out(transistor_3_out), .gate(in_17));
  Transistor #(.\type ("n")) transistor_100 (.in(1'b0), .out(transistor_5_out), .gate(in_17));
  Transistor #(.\type ("n")) transistor_101 (.in(1'b0), .out(transistor_7_out), .gate(in_17));
  Transistor #(.\type ("n")) transistor_102 (.in(1'b0), .out(transistor_8_out), .gate(in_17));
  Transistor #(.\type ("n")) transistor_103 (.in(1'b0), .out(transistor_9_out), .gate(in_17));
  Pull_Resistor #(.pull(1)) pull_resistor_1 (.node(transistor_1_out));
  Pull_Resistor #(.pull(1)) pull_resistor_2 (.node(transistor_2_out));
  Pull_Resistor #(.pull(1)) pull_resistor_3 (.node(transistor_26_out));
  Pull_Resistor #(.pull(1)) pull_resistor_4 (.node(transistor_3_out));
  Pull_Resistor #(.pull(1)) pull_resistor_5 (.node(transistor_4_out));
  Pull_Resistor #(.pull(1)) pull_resistor_6 (.node(transistor_15_out));
  Pull_Resistor #(.pull(1)) pull_resistor_7 (.node(transistor_16_out));
  Pull_Resistor #(.pull(1)) pull_resistor_8 (.node(transistor_5_out));
  Pull_Resistor #(.pull(1)) pull_resistor_9 (.node(transistor_7_out));
  Pull_Resistor #(.pull(1)) pull_resistor_10 (.node(transistor_21_out));
  Pull_Resistor #(.pull(1)) pull_resistor_11 (.node(transistor_8_out));
  Pull_Resistor #(.pull(1)) pull_resistor_12 (.node(transistor_9_out));
endmodule

module SEL_16x12_B (
  input  PCLK,
  input  in_2,
  input  in_3,
  input  in_4,
  input  in_5,
  input  in_6,
  input  in_7,
  input  in_8,
  input  in_9,
  input  in_10,
  input  in_11,
  input  in_12,
  input  in_13,
  input  in_14,
  input  in_15,
  input  in_16,
  input  in_17,
  output out_18,
  output out_19,
  output out_20,
  output out_21,
  output out_22,
  output out_23,
  output out_24,
  output out_25,
  output out_26,
  output out_27,
  output out_28,
  output out_29
);

  wire not_1_out, transistor_1_out, transistor_2_out, transistor_3_out, transistor_4_out, transistor_6_out,
       transistor_7_out, transistor_8_out, transistor_10_out, transistor_13_out, transistor_14_out,
       transistor_18_out, transistor_20_out;

  not not_1 (not_1_out, PCLK);
  and and_1 (out_18, not_1_out, transistor_1_out);
  and and_2 (out_19, not_1_out, transistor_10_out);
  and and_3 (out_20, not_1_out, transistor_2_out);
  and and_4 (out_21, not_1_out, transistor_3_out);
  and and_5 (out_22, not_1_out, transistor_4_out);
  and and_6 (out_23, not_1_out, transistor_13_out);
  and and_7 (out_24, not_1_out, transistor_14_out);
  and and_8 (out_25, not_1_out, transistor_6_out);
  and and_9 (out_26, not_1_out, transistor_7_out);
  and and_10 (out_27, not_1_out, transistor_18_out);
  and and_11 (out_28, not_1_out, transistor_20_out);
  and and_12 (out_29, not_1_out, transistor_8_out);
  Transistor #(.\type ("n")) transistor_1 (.in(1'b0), .out(transistor_1_out), .gate(in_3));
  Transistor #(.\type ("n")) transistor_2 (.in(1'b0), .out(transistor_2_out), .gate(in_2));
  Transistor #(.\type ("n")) transistor_3 (.in(1'b0), .out(transistor_3_out), .gate(in_3));
  Transistor #(.\type ("n")) transistor_4 (.in(1'b0), .out(transistor_4_out), .gate(in_3));
  Transistor #(.\type ("n")) transistor_5 (.in(1'b0), .out(transistor_4_out), .gate(in_2));
  Transistor #(.\type ("n")) transistor_6 (.in(1'b0), .out(transistor_6_out), .gate(in_3));
  Transistor #(.\type ("n")) transistor_7 (.in(1'b0), .out(transistor_7_out), .gate(in_3));
  Transistor #(.\type ("n")) transistor_8 (.in(1'b0), .out(transistor_8_out), .gate(in_3));
  Transistor #(.\type ("n")) transistor_9 (.in(1'b0), .out(transistor_1_out), .gate(in_4));
  Transistor #(.\type ("n")) transistor_10 (.in(1'b0), .out(transistor_10_out), .gate(in_4));
  Transistor #(.\type ("n")) transistor_11 (.in(1'b0), .out(transistor_2_out), .gate(in_5));
  Transistor #(.\type ("n")) transistor_12 (.in(1'b0), .out(transistor_4_out), .gate(in_4));
  Transistor #(.\type ("n")) transistor_13 (.in(1'b0), .out(transistor_13_out), .gate(in_4));
  Transistor #(.\type ("n")) transistor_14 (.in(1'b0), .out(transistor_14_out), .gate(in_4));
  Transistor #(.\type ("n")) transistor_15 (.in(1'b0), .out(transistor_6_out), .gate(in_4));
  Transistor #(.\type ("n")) transistor_16 (.in(1'b0), .out(transistor_6_out), .gate(in_5));
  Transistor #(.\type ("n")) transistor_17 (.in(1'b0), .out(transistor_7_out), .gate(in_4));
  Transistor #(.\type ("n")) transistor_18 (.in(1'b0), .out(transistor_18_out), .gate(in_5));
  Transistor #(.\type ("n")) transistor_19 (.in(1'b0), .out(transistor_18_out), .gate(in_4));
  Transistor #(.\type ("n")) transistor_20 (.in(1'b0), .out(transistor_20_out), .gate(in_4));
  Transistor #(.\type ("n")) transistor_21 (.in(1'b0), .out(transistor_8_out), .gate(in_5));
  Transistor #(.\type ("n")) transistor_22 (.in(1'b0), .out(transistor_8_out), .gate(in_4));
  Transistor #(.\type ("n")) transistor_23 (.in(1'b0), .out(transistor_2_out), .gate(in_6));
  Transistor #(.\type ("n")) transistor_24 (.in(1'b0), .out(transistor_13_out), .gate(in_6));
  Transistor #(.\type ("n")) transistor_25 (.in(1'b0), .out(transistor_18_out), .gate(in_6));
  Transistor #(.\type ("n")) transistor_26 (.in(1'b0), .out(transistor_1_out), .gate(in_7));
  Transistor #(.\type ("n")) transistor_27 (.in(1'b0), .out(transistor_10_out), .gate(in_7));
  Transistor #(.\type ("n")) transistor_28 (.in(1'b0), .out(transistor_2_out), .gate(in_8));
  Transistor #(.\type ("n")) transistor_29 (.in(1'b0), .out(transistor_2_out), .gate(in_7));
  Transistor #(.\type ("n")) transistor_30 (.in(1'b0), .out(transistor_3_out), .gate(in_8));
  Transistor #(.\type ("n")) transistor_31 (.in(1'b0), .out(transistor_3_out), .gate(in_7));
  Transistor #(.\type ("n")) transistor_32 (.in(1'b0), .out(transistor_13_out), .gate(in_7));
  Transistor #(.\type ("n")) transistor_33 (.in(1'b0), .out(transistor_14_out), .gate(in_8));
  Transistor #(.\type ("n")) transistor_34 (.in(1'b0), .out(transistor_14_out), .gate(in_7));
  Transistor #(.\type ("n")) transistor_35 (.in(1'b0), .out(transistor_6_out), .gate(in_7));
  Transistor #(.\type ("n")) transistor_36 (.in(1'b0), .out(transistor_7_out), .gate(in_8));
  Transistor #(.\type ("n")) transistor_37 (.in(1'b0), .out(transistor_18_out), .gate(in_8));
  Transistor #(.\type ("n")) transistor_38 (.in(1'b0), .out(transistor_18_out), .gate(in_7));
  Transistor #(.\type ("n")) transistor_39 (.in(1'b0), .out(transistor_20_out), .gate(in_8));
  Transistor #(.\type ("n")) transistor_40 (.in(1'b0), .out(transistor_20_out), .gate(in_7));
  Transistor #(.\type ("n")) transistor_41 (.in(1'b0), .out(transistor_8_out), .gate(in_7));
  Transistor #(.\type ("n")) transistor_42 (.in(1'b0), .out(transistor_10_out), .gate(in_9));
  Transistor #(.\type ("n")) transistor_43 (.in(1'b0), .out(transistor_3_out), .gate(in_9));
  Transistor #(.\type ("n")) transistor_44 (.in(1'b0), .out(transistor_4_out), .gate(in_9));
  Transistor #(.\type ("n")) transistor_45 (.in(1'b0), .out(transistor_13_out), .gate(in_9));
  Transistor #(.\type ("n")) transistor_46 (.in(1'b0), .out(transistor_6_out), .gate(in_9));
  Transistor #(.\type ("n")) transistor_47 (.in(1'b0), .out(transistor_18_out), .gate(in_9));
  Transistor #(.\type ("n")) transistor_48 (.in(1'b0), .out(transistor_8_out), .gate(in_9));
  Transistor #(.\type ("n")) transistor_49 (.in(1'b0), .out(transistor_1_out), .gate(in_10));
  Transistor #(.\type ("n")) transistor_50 (.in(1'b0), .out(transistor_10_out), .gate(in_11));
  Transistor #(.\type ("n")) transistor_51 (.in(1'b0), .out(transistor_10_out), .gate(in_10));
  Transistor #(.\type ("n")) transistor_52 (.in(1'b0), .out(transistor_2_out), .gate(in_10));
  Transistor #(.\type ("n")) transistor_53 (.in(1'b0), .out(transistor_2_out), .gate(in_11));
  Transistor #(.\type ("n")) transistor_54 (.in(1'b0), .out(transistor_3_out), .gate(in_11));
  Transistor #(.\type ("n")) transistor_55 (.in(1'b0), .out(transistor_4_out), .gate(in_10));
  Transistor #(.\type ("n")) transistor_56 (.in(1'b0), .out(transistor_13_out), .gate(in_10));
  Transistor #(.\type ("n")) transistor_57 (.in(1'b0), .out(transistor_13_out), .gate(in_11));
  Transistor #(.\type ("n")) transistor_58 (.in(1'b0), .out(transistor_14_out), .gate(in_11));
  Transistor #(.\type ("n")) transistor_59 (.in(1'b0), .out(transistor_6_out), .gate(in_11));
  Transistor #(.\type ("n")) transistor_60 (.in(1'b0), .out(transistor_7_out), .gate(in_10));
  Transistor #(.\type ("n")) transistor_61 (.in(1'b0), .out(transistor_18_out), .gate(in_11));
  Transistor #(.\type ("n")) transistor_62 (.in(1'b0), .out(transistor_20_out), .gate(in_11));
  Transistor #(.\type ("n")) transistor_63 (.in(1'b0), .out(transistor_1_out), .gate(in_13));
  Transistor #(.\type ("n")) transistor_64 (.in(1'b0), .out(transistor_10_out), .gate(in_12));
  Transistor #(.\type ("n")) transistor_65 (.in(1'b0), .out(transistor_2_out), .gate(in_13));
  Transistor #(.\type ("n")) transistor_66 (.in(1'b0), .out(transistor_3_out), .gate(in_12));
  Transistor #(.\type ("n")) transistor_67 (.in(1'b0), .out(transistor_4_out), .gate(in_13));
  Transistor #(.\type ("n")) transistor_68 (.in(1'b0), .out(transistor_13_out), .gate(in_13));
  Transistor #(.\type ("n")) transistor_69 (.in(1'b0), .out(transistor_14_out), .gate(in_13));
  Transistor #(.\type ("n")) transistor_70 (.in(1'b0), .out(transistor_6_out), .gate(in_12));
  Transistor #(.\type ("n")) transistor_71 (.in(1'b0), .out(transistor_7_out), .gate(in_13));
  Transistor #(.\type ("n")) transistor_72 (.in(1'b0), .out(transistor_18_out), .gate(in_13));
  Transistor #(.\type ("n")) transistor_73 (.in(1'b0), .out(transistor_20_out), .gate(in_13));
  Transistor #(.\type ("n")) transistor_74 (.in(1'b0), .out(transistor_8_out), .gate(in_12));
  Transistor #(.\type ("n")) transistor_75 (.in(1'b0), .out(transistor_8_out), .gate(in_13));
  Transistor #(.\type ("n")) transistor_76 (.in(1'b0), .out(transistor_10_out), .gate(in_14));
  Transistor #(.\type ("n")) transistor_77 (.in(1'b0), .out(transistor_2_out), .gate(in_14));
  Transistor #(.\type ("n")) transistor_78 (.in(1'b0), .out(transistor_13_out), .gate(in_14));
  Transistor #(.\type ("n")) transistor_79 (.in(1'b0), .out(transistor_18_out), .gate(in_14));
  Transistor #(.\type ("n")) transistor_80 (.in(1'b0), .out(transistor_20_out), .gate(in_14));
  Transistor #(.\type ("n")) transistor_81 (.in(1'b0), .out(transistor_1_out), .gate(in_15));
  Transistor #(.\type ("n")) transistor_82 (.in(1'b0), .out(transistor_1_out), .gate(in_16));
  Transistor #(.\type ("n")) transistor_83 (.in(1'b0), .out(transistor_10_out), .gate(in_16));
  Transistor #(.\type ("n")) transistor_84 (.in(1'b0), .out(transistor_10_out), .gate(in_15));
  Transistor #(.\type ("n")) transistor_85 (.in(1'b0), .out(transistor_2_out), .gate(in_15));
  Transistor #(.\type ("n")) transistor_86 (.in(1'b0), .out(transistor_3_out), .gate(in_16));
  Transistor #(.\type ("n")) transistor_87 (.in(1'b0), .out(transistor_3_out), .gate(in_15));
  Transistor #(.\type ("n")) transistor_88 (.in(1'b0), .out(transistor_13_out), .gate(in_15));
  Transistor #(.\type ("n")) transistor_89 (.in(1'b0), .out(transistor_13_out), .gate(in_16));
  Transistor #(.\type ("n")) transistor_90 (.in(1'b0), .out(transistor_14_out), .gate(in_15));
  Transistor #(.\type ("n")) transistor_91 (.in(1'b0), .out(transistor_6_out), .gate(in_16));
  Transistor #(.\type ("n")) transistor_92 (.in(1'b0), .out(transistor_6_out), .gate(in_15));
  Transistor #(.\type ("n")) transistor_93 (.in(1'b0), .out(transistor_7_out), .gate(in_15));
  Transistor #(.\type ("n")) transistor_94 (.in(1'b0), .out(transistor_18_out), .gate(in_16));
  Transistor #(.\type ("n")) transistor_95 (.in(1'b0), .out(transistor_18_out), .gate(in_15));
  Transistor #(.\type ("n")) transistor_96 (.in(1'b0), .out(transistor_20_out), .gate(in_15));
  Transistor #(.\type ("n")) transistor_97 (.in(1'b0), .out(transistor_8_out), .gate(in_15));
  Transistor #(.\type ("n")) transistor_98 (.in(1'b0), .out(transistor_1_out), .gate(in_17));
  Transistor #(.\type ("n")) transistor_99 (.in(1'b0), .out(transistor_2_out), .gate(in_17));
  Transistor #(.\type ("n")) transistor_100 (.in(1'b0), .out(transistor_14_out), .gate(in_17));
  Transistor #(.\type ("n")) transistor_101 (.in(1'b0), .out(transistor_7_out), .gate(in_17));
  Transistor #(.\type ("n")) transistor_102 (.in(1'b0), .out(transistor_18_out), .gate(in_17));
  Transistor #(.\type ("n")) transistor_103 (.in(1'b0), .out(transistor_20_out), .gate(in_17));
  Pull_Resistor #(.pull(1)) pull_resistor_1 (.node(transistor_1_out));
  Pull_Resistor #(.pull(1)) pull_resistor_2 (.node(transistor_10_out));
  Pull_Resistor #(.pull(1)) pull_resistor_3 (.node(transistor_2_out));
  Pull_Resistor #(.pull(1)) pull_resistor_4 (.node(transistor_3_out));
  Pull_Resistor #(.pull(1)) pull_resistor_5 (.node(transistor_4_out));
  Pull_Resistor #(.pull(1)) pull_resistor_6 (.node(transistor_13_out));
  Pull_Resistor #(.pull(1)) pull_resistor_7 (.node(transistor_14_out));
  Pull_Resistor #(.pull(1)) pull_resistor_8 (.node(transistor_6_out));
  Pull_Resistor #(.pull(1)) pull_resistor_9 (.node(transistor_7_out));
  Pull_Resistor #(.pull(1)) pull_resistor_10 (.node(transistor_18_out));
  Pull_Resistor #(.pull(1)) pull_resistor_11 (.node(transistor_20_out));
  Pull_Resistor #(.pull(1)) pull_resistor_12 (.node(transistor_8_out));
endmodule

module SEL4x16 (
  input  PCLK,
  input  L0,
  input  L1,
  input  C2,
  input  C3,
  output _15,
  output _14,
  output _13,
  output _12,
  output _11,
  output _10,
  output _9,
  output _8,
  output _7,
  output _6,
  output _5,
  output _4,
  output _3,
  output _2,
  output _1,
  output _0
);

  wire not_1_out, not_2_out, not_3_out, not_4_out, not_5_out, transistor_1_out, transistor_5_out,
       transistor_9_out, transistor_13_out, transistor_17_out, transistor_18_out, transistor_25_out,
       transistor_29_out, transistor_33_out, transistor_37_out, transistor_41_out, transistor_45_out,
       transistor_49_out, transistor_50_out, transistor_57_out, transistor_61_out;

  not not_1 (not_1_out, PCLK);
  not not_2 (not_2_out, L0);
  not not_3 (not_3_out, L1);
  not not_4 (not_4_out, C2);
  not not_5 (not_5_out, C3);
  and and_1 (_15, not_1_out, transistor_1_out);
  Transistor #(.\type ("n")) transistor_1 (.in(1'b0), .out(transistor_1_out), .gate(not_2_out));
  Transistor #(.\type ("n")) transistor_2 (.in(1'b0), .out(transistor_1_out), .gate(not_3_out));
  Transistor #(.\type ("n")) transistor_3 (.in(1'b0), .out(transistor_1_out), .gate(not_4_out));
  Transistor #(.\type ("n")) transistor_4 (.in(1'b0), .out(transistor_1_out), .gate(not_5_out));
  Pull_Resistor #(.pull(1)) pull_resistor_1 (.node(transistor_1_out));
  and and_2 (_14, not_1_out, transistor_5_out);
  Transistor #(.\type ("n")) transistor_5 (.in(1'b0), .out(transistor_5_out), .gate(not_2_out));
  Transistor #(.\type ("n")) transistor_6 (.in(1'b0), .out(transistor_5_out), .gate(not_3_out));
  Transistor #(.\type ("n")) transistor_7 (.in(1'b0), .out(transistor_5_out), .gate(C2));
  Transistor #(.\type ("n")) transistor_8 (.in(1'b0), .out(transistor_5_out), .gate(not_5_out));
  Pull_Resistor #(.pull(1)) pull_resistor_2 (.node(transistor_5_out));
  and and_3 (_13, not_1_out, transistor_9_out);
  Transistor #(.\type ("n")) transistor_9 (.in(1'b0), .out(transistor_9_out), .gate(not_2_out));
  Transistor #(.\type ("n")) transistor_10 (.in(1'b0), .out(transistor_9_out), .gate(not_3_out));
  Transistor #(.\type ("n")) transistor_11 (.in(1'b0), .out(transistor_9_out), .gate(not_4_out));
  Transistor #(.\type ("n")) transistor_12 (.in(1'b0), .out(transistor_9_out), .gate(C3));
  Pull_Resistor #(.pull(1)) pull_resistor_3 (.node(transistor_9_out));
  and and_4 (_12, not_1_out, transistor_13_out);
  and and_5 (_11, not_1_out, transistor_17_out);
  Transistor #(.\type ("n")) transistor_13 (.in(1'b0), .out(transistor_13_out), .gate(not_2_out));
  Transistor #(.\type ("n")) transistor_14 (.in(1'b0), .out(transistor_13_out), .gate(not_3_out));
  Transistor #(.\type ("n")) transistor_15 (.in(1'b0), .out(transistor_13_out), .gate(C2));
  Transistor #(.\type ("n")) transistor_16 (.in(1'b0), .out(transistor_13_out), .gate(C3));
  Pull_Resistor #(.pull(1)) pull_resistor_4 (.node(transistor_13_out));
  and and_6 (_10, not_1_out, transistor_18_out);
  Transistor #(.\type ("n")) transistor_17 (.in(1'b0), .out(transistor_17_out), .gate(L0));
  Transistor #(.\type ("n")) transistor_18 (.in(1'b0), .out(transistor_18_out), .gate(L0));
  Transistor #(.\type ("n")) transistor_19 (.in(1'b0), .out(transistor_17_out), .gate(not_3_out));
  Transistor #(.\type ("n")) transistor_20 (.in(1'b0), .out(transistor_18_out), .gate(not_3_out));
  Transistor #(.\type ("n")) transistor_21 (.in(1'b0), .out(transistor_18_out), .gate(C2));
  Transistor #(.\type ("n")) transistor_22 (.in(1'b0), .out(transistor_17_out), .gate(not_4_out));
  Transistor #(.\type ("n")) transistor_23 (.in(1'b0), .out(transistor_18_out), .gate(not_5_out));
  Transistor #(.\type ("n")) transistor_24 (.in(1'b0), .out(transistor_17_out), .gate(not_5_out));
  Pull_Resistor #(.pull(1)) pull_resistor_5 (.node(transistor_17_out));
  Pull_Resistor #(.pull(1)) pull_resistor_6 (.node(transistor_18_out));
  and and_7 (_9, not_1_out, transistor_25_out);
  Transistor #(.\type ("n")) transistor_25 (.in(1'b0), .out(transistor_25_out), .gate(L0));
  Transistor #(.\type ("n")) transistor_26 (.in(1'b0), .out(transistor_25_out), .gate(not_3_out));
  Transistor #(.\type ("n")) transistor_27 (.in(1'b0), .out(transistor_25_out), .gate(not_4_out));
  Transistor #(.\type ("n")) transistor_28 (.in(1'b0), .out(transistor_25_out), .gate(C3));
  Pull_Resistor #(.pull(1)) pull_resistor_7 (.node(transistor_25_out));
  and and_8 (_8, not_1_out, transistor_29_out);
  Transistor #(.\type ("n")) transistor_29 (.in(1'b0), .out(transistor_29_out), .gate(L0));
  Transistor #(.\type ("n")) transistor_30 (.in(1'b0), .out(transistor_29_out), .gate(not_3_out));
  Transistor #(.\type ("n")) transistor_31 (.in(1'b0), .out(transistor_29_out), .gate(C2));
  Transistor #(.\type ("n")) transistor_32 (.in(1'b0), .out(transistor_29_out), .gate(C3));
  Pull_Resistor #(.pull(1)) pull_resistor_8 (.node(transistor_29_out));
  and and_9 (_7, not_1_out, transistor_33_out);
  Transistor #(.\type ("n")) transistor_33 (.in(1'b0), .out(transistor_33_out), .gate(not_2_out));
  Transistor #(.\type ("n")) transistor_34 (.in(1'b0), .out(transistor_33_out), .gate(L1));
  Transistor #(.\type ("n")) transistor_35 (.in(1'b0), .out(transistor_33_out), .gate(not_4_out));
  Transistor #(.\type ("n")) transistor_36 (.in(1'b0), .out(transistor_33_out), .gate(not_5_out));
  Pull_Resistor #(.pull(1)) pull_resistor_9 (.node(transistor_33_out));
  and and_10 (_6, not_1_out, transistor_37_out);
  Transistor #(.\type ("n")) transistor_37 (.in(1'b0), .out(transistor_37_out), .gate(not_2_out));
  Transistor #(.\type ("n")) transistor_38 (.in(1'b0), .out(transistor_37_out), .gate(L1));
  Transistor #(.\type ("n")) transistor_39 (.in(1'b0), .out(transistor_37_out), .gate(C2));
  Transistor #(.\type ("n")) transistor_40 (.in(1'b0), .out(transistor_37_out), .gate(not_5_out));
  Pull_Resistor #(.pull(1)) pull_resistor_10 (.node(transistor_37_out));
  and and_11 (_5, not_1_out, transistor_41_out);
  Transistor #(.\type ("n")) transistor_41 (.in(1'b0), .out(transistor_41_out), .gate(not_2_out));
  Transistor #(.\type ("n")) transistor_42 (.in(1'b0), .out(transistor_41_out), .gate(L1));
  Transistor #(.\type ("n")) transistor_43 (.in(1'b0), .out(transistor_41_out), .gate(not_4_out));
  Transistor #(.\type ("n")) transistor_44 (.in(1'b0), .out(transistor_41_out), .gate(C3));
  Pull_Resistor #(.pull(1)) pull_resistor_11 (.node(transistor_41_out));
  and and_12 (_4, not_1_out, transistor_45_out);
  and and_13 (_3, not_1_out, transistor_50_out);
  Transistor #(.\type ("n")) transistor_45 (.in(1'b0), .out(transistor_45_out), .gate(not_2_out));
  Transistor #(.\type ("n")) transistor_46 (.in(1'b0), .out(transistor_45_out), .gate(L1));
  Transistor #(.\type ("n")) transistor_47 (.in(1'b0), .out(transistor_45_out), .gate(C2));
  Transistor #(.\type ("n")) transistor_48 (.in(1'b0), .out(transistor_45_out), .gate(C3));
  Pull_Resistor #(.pull(1)) pull_resistor_12 (.node(transistor_45_out));
  and and_14 (_2, not_1_out, transistor_49_out);
  Transistor #(.\type ("n")) transistor_49 (.in(1'b0), .out(transistor_49_out), .gate(L0));
  Transistor #(.\type ("n")) transistor_50 (.in(1'b0), .out(transistor_50_out), .gate(L0));
  Transistor #(.\type ("n")) transistor_51 (.in(1'b0), .out(transistor_50_out), .gate(L1));
  Transistor #(.\type ("n")) transistor_52 (.in(1'b0), .out(transistor_49_out), .gate(L1));
  Transistor #(.\type ("n")) transistor_53 (.in(1'b0), .out(transistor_49_out), .gate(C2));
  Transistor #(.\type ("n")) transistor_54 (.in(1'b0), .out(transistor_50_out), .gate(not_4_out));
  Transistor #(.\type ("n")) transistor_55 (.in(1'b0), .out(transistor_50_out), .gate(not_5_out));
  Transistor #(.\type ("n")) transistor_56 (.in(1'b0), .out(transistor_49_out), .gate(not_5_out));
  Pull_Resistor #(.pull(1)) pull_resistor_13 (.node(transistor_49_out));
  Pull_Resistor #(.pull(1)) pull_resistor_14 (.node(transistor_50_out));
  and and_15 (_1, not_1_out, transistor_57_out);
  Transistor #(.\type ("n")) transistor_57 (.in(1'b0), .out(transistor_57_out), .gate(L0));
  Transistor #(.\type ("n")) transistor_58 (.in(1'b0), .out(transistor_57_out), .gate(L1));
  Transistor #(.\type ("n")) transistor_59 (.in(1'b0), .out(transistor_57_out), .gate(not_4_out));
  Transistor #(.\type ("n")) transistor_60 (.in(1'b0), .out(transistor_57_out), .gate(C3));
  Pull_Resistor #(.pull(1)) pull_resistor_15 (.node(transistor_57_out));
  and and_16 (_0, not_1_out, transistor_61_out);
  Transistor #(.\type ("n")) transistor_61 (.in(1'b0), .out(transistor_61_out), .gate(L0));
  Transistor #(.\type ("n")) transistor_62 (.in(1'b0), .out(transistor_61_out), .gate(L1));
  Transistor #(.\type ("n")) transistor_63 (.in(1'b0), .out(transistor_61_out), .gate(C2));
  Transistor #(.\type ("n")) transistor_64 (.in(1'b0), .out(transistor_61_out), .gate(C3));
  Pull_Resistor #(.pull(1)) pull_resistor_16 (.node(transistor_61_out));
endmodule
