// Logisim project CounterStage.circ as structural Verilog: 3 circuits, main circuit main
module main (
  input  CLR,
  input  CLK,
  input  ncarry_in,
  input  RES,
  output out,
  output ncarry_out,
  output ff,
  output latch
);

  wire multiplexer_1_out, nor_3_out, not_1_out, not_2_out, not_3_out;

  not not_1 (not_1_out, CLK);
  Multiplexer multiplexer_1 (.in0(not_2_out), .in1(out), .out(multiplexer_1_out), .sel(ncarry_in));  // open: en
  not not_2 (not_2_out, ff);
  Multiplexer multiplexer_2 (.in0(out), .in1(nor_3_out), .out(ff), .sel(CLK));  // open: en
  not not_3 (not_3_out, ncarry_in);
  nor nor_1 (out, not_2_out, RES);
  nor nor_2 (ncarry_out, not_2_out, not_3_out);
  nor nor_3 (nor_3_out, latch, CLR);
  DLatch DLatch (.EN(not_1_out), .D(multiplexer_1_out), .Q(latch));  // open: NOT_Q

  // Notes on the sheet:
  //   clear manually
  //   global RESET
  //   FF
endmodule

module DLatch (
  input  EN,
  input  D,
  output Q,
  output NOT_Q
);

  D_Flip_Flop #(.trigger("high")) d_ff_1 (.clk(EN), .D(D), .Q(Q), .Qn(NOT_Q));  // open: preset, en, reset
endmodule

module _2BitCounter (
  input  CLR,
  input  RES,
  input  nCarry_In,
  output Bit_0,
  output Bit_1
);

  wire main_1_ncarry_out, PCLK_out;

  Clock PCLK (.out(PCLK_out));
  main main_1 (
    .CLR(CLR), .CLK(PCLK_out), .ncarry_in(nCarry_In), .RES(RES), .out(Bit_0), .ncarry_out(main_1_ncarry_out));  // open: ff, latch
  main main_2 (
    .CLR(CLR), .CLK(PCLK_out), .ncarry_in(main_1_ncarry_out), .RES(RES), .out(Bit_1));  // open: ncarry_out, ff, latch
endmodule
