// Logisim project HV_FSM_Standalone_Evo.circ as structural Verilog
module HV_FSM (
);

  DelayedH DelayedH_inst ();  // open: H5_DashDash, H4_DashDash, H3_DashDash, H2_DashDash, n_H2_Dash, H1_DashDash, n_H1_Dash, H0_DashDash, H0_Dash, PCLK, n_PCLK, H_Input
  EvenOdd EvenOdd_inst ();  // open: EvenOddOut, RES, n_HPLA_5, RESCL, V8
  VBlankInterrupt VB_Intr_inst ();  // open: INT, DB7_Out, n_VSET, VBL, RESCL, n_R2, n_DBE, PCLK, n_PCLK
  HVCountersControl hvcounterscontrol_1 ();  // open: HC, VC, V_IN, HPLA_23, EvenOddOut, VPLA_2, n_PCLK
endmodule

module DLatch (
  input  Enable,
  input  Value,
  output ValOut,
  output n_ValOut
);

  D_Flip_Flop #(.trigger("high")) d_ff_1 (.D(Value), .clk(Enable), .Q(ValOut), .Qn(n_ValOut));  // open: preset, reset
endmodule

module DelayedH (
  input  PCLK,
  input  n_PCLK,
  input  [8:0] H_Input,
  output H5_DashDash,
  output H4_DashDash,
  output H3_DashDash,
  output H2_DashDash,
  output n_H2_Dash,
  output H1_DashDash,
  output n_H1_Dash,
  output H0_DashDash,
  output H0_Dash
);

  wire h0_latch1_n_valout, h0_latch2_n_valout, h2_latch1_n_valout, h3_latch1_n_valout, h4_latch1_n_valout,
       h5_latch1_n_valout;

  DLatch h5_latch1 (.n_ValOut(h5_latch1_n_valout), .Enable(n_PCLK), .Value(H_Input[5]));  // open: ValOut
  DLatch h4_latch1 (.n_ValOut(h4_latch1_n_valout), .Enable(n_PCLK), .Value(H_Input[4]));  // open: ValOut
  DLatch h3_latch1 (.n_ValOut(h3_latch1_n_valout), .Enable(n_PCLK), .Value(H_Input[3]));  // open: ValOut
  DLatch h2_latch1 (.n_ValOut(h2_latch1_n_valout), .Enable(n_PCLK), .Value(H_Input[2]));  // open: ValOut
  DLatch h1_latch1 (.n_ValOut(n_H1_Dash), .Enable(n_PCLK), .Value(H_Input[1]));  // open: ValOut
  DLatch h0_latch1 (.n_ValOut(h0_latch1_n_valout), .Enable(n_PCLK), .Value(H_Input[0]));  // open: ValOut
  DLatch h5_latch2 (.n_ValOut(H5_DashDash), .Enable(PCLK), .Value(h5_latch1_n_valout));  // open: ValOut
  DLatch h4_latch2 (.n_ValOut(H4_DashDash), .Enable(PCLK), .Value(h4_latch1_n_valout));  // open: ValOut
  DLatch h3_latch2 (.n_ValOut(H3_DashDash), .Enable(PCLK), .Value(h3_latch1_n_valout));  // open: ValOut
  DLatch h2_latch2 (.n_ValOut(H2_DashDash), .Enable(PCLK), .Value(h2_latch1_n_valout));  // open: ValOut
  DLatch h1_latch2 (.n_ValOut(H1_DashDash), .Enable(PCLK), .Value(n_H1_Dash));  // open: ValOut
  DLatch h0_latch2 (.n_ValOut(h0_latch2_n_valout), .Enable(PCLK), .Value(h0_latch1_n_valout));  // open: ValOut
  buf buffer_1 (n_H2_Dash, h2_latch1_n_valout);
  buf buffer_2 (H0_DashDash, h0_latch2_n_valout);
  not not_1 (H0_Dash, h0_latch1_n_valout);
endmodule

module EvenOdd (
  input  V8,
  input  RES,
  input  n_HPLA_5,
  input  RESCL,
  output EvenOddOut
);

  wire multiplexer_1_out, multiplexer_2_out, nor_1_out, not_1_out, not_2_out, not_3_out, not_4_out;

  not not_1 (not_1_out, multiplexer_1_out);
  Multiplexer multiplexer_1 (.in0(not_3_out), .in1(not_2_out), .out(multiplexer_1_out), .sel(V8));
  not not_2 (not_2_out, not_1_out);
  Multiplexer multiplexer_2 (.in0(nor_1_out), .in1(not_2_out), .out(multiplexer_2_out), .sel(V8));
  not not_3 (not_3_out, multiplexer_2_out);
  nor nor_1 (nor_1_out, RES, not_3_out);
  not not_4 (not_4_out, RESCL);
  nor nor_2 (EvenOddOut, nor_1_out, n_HPLA_5, not_4_out);

  // Notes on the sheet:
  //   FF_1
  //   FF_2
endmodule

module HVCountersControl (
  input  n_PCLK,
  input  HPLA_23,
  input  EvenOddOut,
  input  VPLA_2,
  output V_IN,
  output HC,
  output VC
);

  wire ctrl_latch2_n_valout, nor_1_out, not_1_out;

  DLatch ctrl_latch1 (.n_ValOut(HC), .Enable(n_PCLK), .Value(nor_1_out));  // open: ValOut
  nor nor_1 (nor_1_out, HPLA_23, EvenOddOut);
  DLatch ctrl_latch2 (.n_ValOut(ctrl_latch2_n_valout), .Enable(n_PCLK), .Value(VPLA_2));  // open: ValOut
  not not_1 (not_1_out, HC);
  nor nor_2 (VC, not_1_out, ctrl_latch2_n_valout);

  assign V_IN = HPLA_23;
endmodule

module VBlankInterrupt (
  input  PCLK,
  input  n_PCLK,
  input  n_VSET,
  input  VBL,
  input  RESCL,
  input  n_R2,
  input  n_DBE,
  output INT,
  output DB7_Out
);

  wire db_latch_n_valout, nor_1_out, nor_2_out, nor_3_out, nor_4_out, not_1_out, not_2_out, not_3_out,
       vset_latch1_valout, vset_latch2_valout;

  DLatch vset_latch1 (.ValOut(vset_latch1_valout), .Enable(PCLK), .Value(n_VSET));  // open: n_ValOut
  nor nor_1 (nor_1_out, n_R2, n_DBE);
  DLatch vset_latch2 (.ValOut(vset_latch2_valout), .Enable(n_PCLK), .Value(vset_latch1_valout));  // open: n_ValOut
  nor nor_2 (nor_2_out, n_PCLK, n_VSET, vset_latch2_valout);
  nor nor_3 (nor_3_out, nor_2_out, nor_4_out);
  nor nor_4 (nor_4_out, nor_3_out, RESCL, nor_1_out);
  not not_1 (not_1_out, nor_4_out);
  not not_2 (not_2_out, VBL);
  nor nor_5 (INT, not_2_out, not_1_out);
  not not_3 (not_3_out, nor_1_out);
  DLatch db_latch (.n_ValOut(db_latch_n_valout), .Enable(not_3_out), .Value(not_1_out));  // open: ValOut
  assign DB7_Out = nor_1_out ? db_latch_n_valout : 1'bz;  // Controlled_Buffer controlled_buffer_1

  // Notes on the sheet:
  //   Read Enabler
  //   Edge Detect
  //   R2_EN
  //   INT_FF
endmodule
