// Logisim project sprite_0_hit.circ as structural Verilog: 1 circuit, main circuit main
module main (
  input  BGC0,
  input  BGC1,
  input  SPR0HIT,
  input  LOL,
  input  PCLK,
  input  nVIS,
  output STRIKE
);

  wire nor_1_out;

  nor nor_1 (nor_1_out, BGC0, BGC1);
  nor nor_2 (STRIKE, nor_1_out, SPR0HIT, LOL, PCLK, nVIS);
endmodule
