// Logisim project 2A03_APU_ForAPUPlayer.circ as structural Verilog: 39 circuits, main circuit 2A03_APU
module _2A03_APU (
  input  DBG__EXT,
  input  CLK,
  input  nNMI_PIN,
  input  nIRQ_PIN,
  input  nRES_PIN,
  input  PHI1_FromCore,
  input  PHI2_FromCore,
  input  R_W__CPU,
  input  [15:0] CPU_Ax,
  input  [7:0] Data_from_CPU,
  input  [7:0] DB_in_EXT,
  output [7:0] AUX_A,
  output [5:0] SQB_ENV,
  output [10:0] SQA_F,
  output [5:0] SQA_ENV,
  output [7:0] SW_A,
  output [1:0] SQA_DUTY,
  output [7:0] SW_B,
  output [10:0] SQB_F,
  output [1:0] SQB_DUTY,
  output [7:0] SAMPLE_LENGTH,
  output DMC,
  output [3:0] DMCF,
  output [10:0] TRI_FREQ,
  output DMC_ENIRQ,
  output DMC_LOOP,
  output [7:0] TRI_LIN,
  output [7:0] SAMPLE_BUF,
  output [7:0] SAMPLE_ADR,
  output OUT0,
  output OUT1,
  output OUT2,
  output nIN0,
  output nIN1,
  output R_W__EXT,
  output M2__EXT,
  output [15:0] AB,
  output [14:0] AUX_B,
  output PHI0__CPU,
  output nIRQ_CPU,
  output [5:0] N_ENV,
  output nNMI_CPU,
  output RND,
  output RMODE,
  output [3:0] N_REQ,
  output TRI,
  output RDY__CPU,
  output [7:0] Data_to_CPU,
  output [7:0] DB_out_EXT,
  output SQB,
  output SQA
);

  wire ACLK, clk_divider_1_nm2, dpcm_channel_1_dmca0, dpcm_channel_1_dmca1, dpcm_channel_1_dmca2,
       dpcm_channel_1_dmca3, dpcm_channel_1_dmca4, dpcm_channel_1_dmca5, dpcm_channel_1_dmca6,
       dpcm_channel_1_dmca7, dpcm_channel_1_dmca8, dpcm_channel_1_dmca9, dpcm_channel_1_dmca10,
       dpcm_channel_1_dmca11, dpcm_channel_1_dmca12, dpcm_channel_1_dmca13, dpcm_channel_1_dmca14,
       dpcm_channel_1_dmcint, dpcm_channel_1_dmcrdy, dpcm_channel_1_ndmc_ab, dpcm_channel_1_rundmc,
       io_control_1_nclk_int, length_down_counter_1_noxxx, length_down_counter_2_noxxx,
       length_down_counter_3_noxxx, length_down_counter_4_noxxx, length_table_1_lc0, length_table_1_lc1,
       length_table_1_lc2, length_table_1_lc3, length_table_1_lc4, length_table_1_lc5, length_table_1_lc6,
       length_table_1_lc7, lfo_1_int, LOCK, nACLK, nDBGRD, nLFO1, nLFO2, noise_channel_1_nrnd_lc, not_3_out,
       not_6_out, not_7_out, not_8_out, not_9_out, not_10_out, nR401A, nR4015, nR4016, nR4017, nR4018,
       nR4019, PHI1, PHI2, RES, sprite_dma_1_r_w__to_r_w_ic_pin, sprite_dma_1_spr_ppu, sprite_dma_1_wr,
       square_channel_0_1_nsqa_lc, square_channel_1_1_nsqb_lc, triangle_channel_1_tri_lc, W400A, W400B,
       W400C, W400E, W400F, W401A, W4000, W4001, W4002, W4003, W4004, W4005, W4006, W4007, W4008, W4010,
       W4011, W4012, W4013, W4014, W4015, W4016, W4017;
  wire [15:0] sprite_dma_1_a0;

  SQUARE_CHANNEL_1 square_channel_1_1 (
    .ACLK(ACLK), .nACLK(nACLK), .W4004(W4004), .W4005(W4005), .W4006(W4006), .W4007(W4007),
    .D0(Data_from_CPU[0]), .D1(Data_from_CPU[1]), .D2(Data_from_CPU[2]), .D3(Data_from_CPU[3]),
    .D4(Data_from_CPU[4]), .D5(Data_from_CPU[5]), .D6(Data_from_CPU[6]), .D7(Data_from_CPU[7]),
    .NOSQB(length_down_counter_3_noxxx), .RES(RES), .nLFO1(nLFO1), .nLFO2(nLFO2), .SQB0(AUX_A[4]),
    .SQB1(AUX_A[5]), .SQB2(AUX_A[6]), .SQB3(AUX_A[7]), .nSQB_LC(square_channel_1_1_nsqb_lc), .LOCK(LOCK),
    .SWEEP_REG(SW_B), .SQB_F(SQB_F), .SQB_ENV(SQB_ENV), .SQB_DUTY(SQB_DUTY));
  TRIANGLE_CHANNEL triangle_channel_1 (
    .PHI1(PHI1), .nACLK(nACLK), .W4008(W4008), .W400A(W400A), .W400B(W400B), .D0(Data_from_CPU[0]),
    .D1(Data_from_CPU[1]), .D2(Data_from_CPU[2]), .D3(Data_from_CPU[3]), .D4(Data_from_CPU[4]),
    .D5(Data_from_CPU[5]), .D6(Data_from_CPU[6]), .D7(Data_from_CPU[7]), .RES(RES), .nLFO1(nLFO1),
    .NOTRI(length_down_counter_2_noxxx), .TRI0(AUX_B[0]), .TRI1(AUX_B[1]), .TRI2(AUX_B[2]), .TRI3(AUX_B[3]),
    .TRI_LC(triangle_channel_1_tri_lc), .LOCk(LOCK), .W401A(W401A), .TRI_FREQ(TRI_FREQ), .TRI_LIN(TRI_LIN));
  NOISE_CHANNEL noise_channel_1 (
    .ACLK(ACLK), .nACLK(nACLK), .D7(Data_from_CPU[7]), .D5(Data_from_CPU[5]), .D4(Data_from_CPU[4]),
    .D3(Data_from_CPU[3]), .D2(Data_from_CPU[2]), .D1(Data_from_CPU[1]), .D0(Data_from_CPU[0]),
    .W400E(W400E), .W400F(W400F), .Res(RES), .NORND(length_down_counter_1_noxxx), .nLFO1(nLFO1),
    .W400C(W400C), .RND0(AUX_B[4]), .RND1(AUX_B[5]), .RND2(AUX_B[6]), .RND3(AUX_B[7]),
    .nRND_LC(noise_channel_1_nrnd_lc), .LOCK(LOCK), .N_ENV(N_ENV), .RMODE(RMODE), .N_FREQ(N_REQ));
  LENGTH_TABLE length_table_1 (
    .D3(Data_from_CPU[3]), .D4(Data_from_CPU[4]), .D5(Data_from_CPU[5]), .D6(Data_from_CPU[6]),
    .D7(Data_from_CPU[7]), .LC7(length_table_1_lc7), .LC6(length_table_1_lc6), .LC5(length_table_1_lc5),
    .LC4(length_table_1_lc4), .LC3(length_table_1_lc3), .LC2(length_table_1_lc2), .LC1(length_table_1_lc1),
    .LC0(length_table_1_lc0));
  not not_1 (RND, length_down_counter_1_noxxx);
  not not_2 (TRI, length_down_counter_2_noxxx);
  not not_3 (not_3_out, ACLK);
  LENGTH_DOWN_COUNTER length_down_counter_1 (
    .nACLK(nACLK), .W400x(W400F), .LC7(length_table_1_lc7), .LC6(length_table_1_lc6),
    .LC5(length_table_1_lc5), .LC4(length_table_1_lc4), .LC3(length_table_1_lc3), .LC2(length_table_1_lc2),
    .LC1(length_table_1_lc1), .LC0(length_table_1_lc0), .HALT(noise_channel_1_nrnd_lc),
    .NOxxx(length_down_counter_1_noxxx), .W4015(W4015), .Dx_2(Data_to_CPU[3]), .Dx(Data_from_CPU[3]),
    .RES(RES), .nLFO2(nLFO2), .nR4015(nR4015), .nACLK4(not_3_out));
  LENGTH_DOWN_COUNTER length_down_counter_2 (
    .nACLK(nACLK), .W400x(W400B), .LC7(length_table_1_lc7), .LC6(length_table_1_lc6),
    .LC5(length_table_1_lc5), .LC4(length_table_1_lc4), .LC3(length_table_1_lc3), .LC2(length_table_1_lc2),
    .LC1(length_table_1_lc1), .LC0(length_table_1_lc0), .HALT(triangle_channel_1_tri_lc),
    .NOxxx(length_down_counter_2_noxxx), .W4015(W4015), .Dx_2(Data_to_CPU[2]), .Dx(Data_from_CPU[2]),
    .RES(RES), .nLFO2(nLFO2), .nR4015(nR4015), .nACLK4(not_3_out));
  SQUARE_CHANNEL_0 square_channel_0_1 (
    .ACLK(ACLK), .nACLK(nACLK), .W4000(W4000), .W4001(W4001), .W4002(W4002), .W4003(W4003),
    .D0(Data_from_CPU[0]), .D1(Data_from_CPU[1]), .D2(Data_from_CPU[2]), .D3(Data_from_CPU[3]),
    .D4(Data_from_CPU[4]), .D5(Data_from_CPU[5]), .D6(Data_from_CPU[6]), .D7(Data_from_CPU[7]),
    .NOSQA(length_down_counter_4_noxxx), .RES(RES), .nLFO1(nLFO1), .nLFO2(nLFO2), .SQA0(AUX_A[0]),
    .SQA1(AUX_A[1]), .SQ2(AUX_A[2]), .SQA3(AUX_A[3]), .nSQA_LC(square_channel_0_1_nsqa_lc), .LOCK(LOCK),
    .SQA_F(SQA_F), .SWEEP_REG(SW_A), .SQA_ENV(SQA_ENV), .SQA_DUTY(SQA_DUTY));
  SPRITE_DMA sprite_dma_1 (
    .PHI1(PHI1), .PHI2(PHI2_FromCore), .ACLK(ACLK), .nACLK(nACLK), .nR4015(nR4015), .W4014(W4014),
    .D0(Data_from_CPU[0]), .D1(Data_from_CPU[1]), .D2(Data_from_CPU[2]), .D3(Data_from_CPU[3]),
    .D4(Data_from_CPU[4]), .D5(Data_from_CPU[5]), .D6(Data_from_CPU[6]), .D7(Data_from_CPU[7]),
    .RUNDMC(dpcm_channel_1_rundmc), .DMC_RDY(dpcm_channel_1_dmcrdy), .nDMC_AB(dpcm_channel_1_ndmc_ab),
    .R_W__CPU(R_W__CPU), .RES(RES), .CPUA0(CPU_Ax[0]), .CPUA1(CPU_Ax[1]), .CPUA2(CPU_Ax[2]),
    .CPUA3(CPU_Ax[3]), .CPUA4(CPU_Ax[4]), .CPUA5(CPU_Ax[5]), .CPUA6(CPU_Ax[6]), .CPUA7(CPU_Ax[7]),
    .CPUA8(CPU_Ax[8]), .CPUA9(CPU_Ax[9]), .CPUA10(CPU_Ax[10]), .CPUA11(CPU_Ax[11]), .CPUA12(CPU_Ax[12]),
    .CPUA13(CPU_Ax[13]), .CPUA14(CPU_Ax[14]), .CPUA15(CPU_Ax[15]), .DMC0(dpcm_channel_1_dmca0),
    .DMC1(dpcm_channel_1_dmca1), .DMC2(dpcm_channel_1_dmca2), .DMC3(dpcm_channel_1_dmca3),
    .DMC4(dpcm_channel_1_dmca4), .DMC5(dpcm_channel_1_dmca5), .DMC6(dpcm_channel_1_dmca6),
    .DMC7(dpcm_channel_1_dmca7), .DMC8(dpcm_channel_1_dmca8), .DMC9(dpcm_channel_1_dmca9),
    .DMC10(dpcm_channel_1_dmca10), .DMC11(dpcm_channel_1_dmca11), .DMC12(dpcm_channel_1_dmca12),
    .DMC13(dpcm_channel_1_dmca13), .DMC14(dpcm_channel_1_dmca14),
    .R_W__to_R_W_ic_pin(sprite_dma_1_r_w__to_r_w_ic_pin), .WR(sprite_dma_1_wr), .RDY(RDY__CPU),
    .A0(sprite_dma_1_a0[0]), .A1(sprite_dma_1_a0[1]), .A2(sprite_dma_1_a0[2]), .A3(sprite_dma_1_a0[3]),
    .A4(sprite_dma_1_a0[4]), .A5(sprite_dma_1_a0[5]), .A6(sprite_dma_1_a0[6]), .A7(sprite_dma_1_a0[7]),
    .A8(sprite_dma_1_a0[8]), .A9(sprite_dma_1_a0[9]), .A10(sprite_dma_1_a0[10]), .A11(sprite_dma_1_a0[11]),
    .A12(sprite_dma_1_a0[12]), .A13(sprite_dma_1_a0[13]), .A14(sprite_dma_1_a0[14]),
    .A15(sprite_dma_1_a0[15]), .D0_3(Data_to_CPU[0]), .D0_2(Data_from_CPU[0]), .D1_3(Data_to_CPU[1]),
    .D1_2(Data_from_CPU[1]), .D2_3(Data_to_CPU[2]), .D2_2(Data_from_CPU[2]), .D3_3(Data_to_CPU[3]),
    .D3_2(Data_from_CPU[3]), .D4_3(Data_to_CPU[4]), .D4_2(Data_from_CPU[4]), .D5_3(Data_to_CPU[5]),
    .D5_2(Data_from_CPU[5]), .D6_3(Data_to_CPU[6]), .D6_2(Data_from_CPU[6]), .D7_3(Data_to_CPU[7]),
    .D7_2(Data_from_CPU[7]), .nDBGRD(nDBGRD), .SPR_PPU(sprite_dma_1_spr_ppu));
  DPCM_CHANNEL dpcm_channel_1 (
    .PHI1(PHI1), .ACLK(ACLK), .nACLK(nACLK), .W4010(W4010), .W4011(W4011), .W4012(W4012), .W4013(W4013),
    .W4015(W4015), .nR4015(nR4015), .D0(Data_from_CPU[0]), .D1(Data_from_CPU[1]), .D2(Data_from_CPU[2]),
    .D3(Data_from_CPU[3]), .D4(Data_from_CPU[4]), .D5(Data_from_CPU[5]), .D6(Data_from_CPU[6]),
    .D7(Data_from_CPU[7]), .R_W(R_W__CPU), .Res(RES), .D4_2(Data_to_CPU[4]), .DMCINT(dpcm_channel_1_dmcint),
    .D7_2(Data_to_CPU[7]), .RUNDMC(dpcm_channel_1_rundmc), .DMCRDY(dpcm_channel_1_dmcrdy),
    .nDMC_AB(dpcm_channel_1_ndmc_ab), .DMC0(AUX_B[8]), .DMC1(AUX_B[9]), .DMC2(AUX_B[10]), .DMC3(AUX_B[11]),
    .DMC4(AUX_B[12]), .DMC5(AUX_B[13]), .DMC6(AUX_B[14]), .DMCA0(dpcm_channel_1_dmca0),
    .DMCA1(dpcm_channel_1_dmca1), .DMCA2(dpcm_channel_1_dmca2), .DMCA3(dpcm_channel_1_dmca3),
    .DMCA4(dpcm_channel_1_dmca4), .DMCA5(dpcm_channel_1_dmca5), .DMCA6(dpcm_channel_1_dmca6),
    .DMCA7(dpcm_channel_1_dmca7), .DMCA8(dpcm_channel_1_dmca8), .DMCA9(dpcm_channel_1_dmca9),
    .DMCA10(dpcm_channel_1_dmca10), .DMCA11(dpcm_channel_1_dmca11), .DMCA12(dpcm_channel_1_dmca12),
    .DMCA13(dpcm_channel_1_dmca13), .DMCA14(dpcm_channel_1_dmca14), .LOCK(LOCK), .DMC_EN(DMC), .DMC_F(DMCF),
    .DMC_ENIRQ(DMC_ENIRQ), .DMC_LOOP(DMC_LOOP), .SAMPLE_LENGTH(SAMPLE_LENGTH), .SAMPLE_ADR(SAMPLE_ADR),
    .SAMPLE_BUF(SAMPLE_BUF));
  LENGTH_DOWN_COUNTER length_down_counter_3 (
    .nACLK(nACLK), .W400x(W4007), .LC7(length_table_1_lc7), .LC6(length_table_1_lc6),
    .LC5(length_table_1_lc5), .LC4(length_table_1_lc4), .LC3(length_table_1_lc3), .LC2(length_table_1_lc2),
    .LC1(length_table_1_lc1), .LC0(length_table_1_lc0), .HALT(square_channel_1_1_nsqb_lc),
    .NOxxx(length_down_counter_3_noxxx), .W4015(W4015), .Dx_2(Data_to_CPU[1]), .Dx(Data_from_CPU[1]),
    .RES(RES), .nLFO2(nLFO2), .nR4015(nR4015), .nACLK4(not_3_out));
  LENGTH_DOWN_COUNTER length_down_counter_4 (
    .nACLK(nACLK), .W400x(W4003), .LC7(length_table_1_lc7), .LC6(length_table_1_lc6),
    .LC5(length_table_1_lc5), .LC4(length_table_1_lc4), .LC3(length_table_1_lc3), .LC2(length_table_1_lc2),
    .LC1(length_table_1_lc1), .LC0(length_table_1_lc0), .HALT(square_channel_0_1_nsqa_lc),
    .NOxxx(length_down_counter_4_noxxx), .W4015(W4015), .Dx_2(Data_to_CPU[0]), .Dx(Data_from_CPU[0]),
    .RES(RES), .nLFO2(nLFO2), .nR4015(nR4015), .nACLK4(not_3_out));
  not not_4 (SQB, length_down_counter_3_noxxx);
  not not_5 (SQA, length_down_counter_4_noxxx);
  D_Flip_Flop #(.trigger("low")) d_ff_1 (
    .clk(not_6_out), .D(Data_from_CPU[7]), .Q(LOCK), .en(W401A), .reset(RES));  // open: Qn, preset
  not not_6 (not_6_out, nACLK);
  REGISTER_SELECT register_select_1 (
    .PHI1(PHI1), .R_W(R_W__CPU), .A15(CPU_Ax[15]), .A14(CPU_Ax[14]), .A13(CPU_Ax[13]), .A12(CPU_Ax[12]),
    .A11(CPU_Ax[11]), .A10(CPU_Ax[10]), .A9(CPU_Ax[9]), .A8(CPU_Ax[8]), .A7(CPU_Ax[7]), .A6(CPU_Ax[6]),
    .A5(CPU_Ax[5]), .A4(sprite_dma_1_a0[4]), .A3(sprite_dma_1_a0[3]), .A2(sprite_dma_1_a0[2]),
    .A1(sprite_dma_1_a0[1]), .A0(sprite_dma_1_a0[0]), .W4000(W4000), .W4001(W4001), .W4002(W4002),
    .W4003(W4003), .W4004(W4004), .W4005(W4005), .W4006(W4006), .W4007(W4007), .W4008(W4008), .W400A(W400A),
    .W400B(W400B), .W400C(W400C), .W400E(W400E), .W400F(W400F), .W4010(W4010), .W4011(W4011), .W4012(W4012),
    .W4013(W4013), .W4014(W4014), .W4015(W4015), .W4016(W4016), .W4017(W4017), .nR4015(nR4015),
    .nR4016(nR4016), .nR4017(nR4017), .nR4018(nR4018), .nR4019(nR4019), .nR401A(nR401A), .W401A(W401A),
    .DBG(DBG__EXT), .nDBGRD(nDBGRD));
  LFO lfo_1 (
    .W4017(W4017), .D7(Data_from_CPU[7]), .D6(Data_from_CPU[6]), .Res(RES), .nR4015(nR4015),
    .DMCINT(dpcm_channel_1_dmcint), .nLFO1(nLFO1), .nLFO2(nLFO2), .INT(lfo_1_int), .D6_State(Data_to_CPU[6]),
    .PHI1(PHI1), .nACLK(nACLK), .ACLK(ACLK));
  ACLK aclk_1 (.PHI0(CLK), .RES(RES), .PHI1(PHI1), .PHI2(PHI2), .ACLK(ACLK), .nACLK(nACLK));
  CLK_DIVIDER clk_divider_1 (
    .nCLK(io_control_1_nclk_int), .PHI2_CPU(PHI2_FromCore), .nM2(clk_divider_1_nm2));  // open: PHI0_CPU
  IO_CONTROL io_control_1 (
    .ACLK(ACLK), .W4016(W4016), .D0(Data_from_CPU[0]), .D1(Data_from_CPU[1]), .D2(Data_from_CPU[2]),
    .nRES_PIN(nRES_PIN), .R_W_int(sprite_dma_1_r_w__to_r_w_ic_pin), .nR4016(nR4016), .nR4017(nR4017),
    .nNMI_INT(nNMI_CPU), .nIRQ_INT(nIRQ_CPU), .INT_from_apu(lfo_1_int), .nCLK_INT(io_control_1_nclk_int),
    .OUT0_PIN(OUT0), .OUT1_PIN(OUT1), .OUT2_PIN(OUT2), .MASTER_RESET(RES), .R_W_PIN(R_W__EXT),
    .IN0_PIN(nIN0), .IN1_PIN(nIN1), .nNMI_PIN(nNMI_PIN), .nIRQ_PIN(nIRQ_PIN), .CLK_PIN(CLK),
    .nM2(clk_divider_1_nm2), .M2(M2__EXT), .DBG(DBG__EXT), .Ax(AB), .APU_Ax(sprite_dma_1_a0),
    .WR(sprite_dma_1_wr), .nACLK(nACLK));  // open: DB_OUT, DB_OUT_EXT, DB_IN, DB_IN_EXT
  not not_7 (not_7_out, not_8_out);
  not not_8 (not_8_out, sprite_dma_1_r_w__to_r_w_ic_pin);
  not not_9 (not_9_out, sprite_dma_1_wr);
  assign DB_out_EXT = not_10_out ? Data_to_CPU : 8'bz;  // Controlled_Buffer controlled_buffer_1
  not not_10 (not_10_out, not_7_out);
  assign Data_from_CPU = not_9_out ? DB_in_EXT : 8'bz;  // Controlled_Buffer controlled_buffer_2

  assign PHI0__CPU = CLK;

  // Other names for the same wires on the sheet: PHI2_CPU = PHI2_FromCore

  // Notes on the sheet:
  //   2A03 APU
  //   DMC[6:0]
  //   LENGTH COUNTER NOISE
  //   LENGTH COUNTER TRIANGLE
  //   LENGTH COUNTER SQUARE 1
  //   LENGTH COUNTER SQUARE 0
  //   LOCK FF
  //   CPU ADDRESS  BUS
  //   CLOCK 6502
  //   RD
  //   EXTERNAL DATA BUS
  //   EXTERNAL ADDRESS BUS
endmodule

module D_latch (
  input  EN,
  input  D,
  output Q,
  output NOT_Q
);

  D_Flip_Flop #(.trigger("high")) d_ff_1 (.clk(EN), .D(D), .Q(Q), .Qn(NOT_Q));  // open: preset, en, reset
endmodule

module LFO (
  input  ACLK,
  input  nACLK,
  input  W4017,
  input  D7,
  input  D6,
  input  Res,
  input  PHI1,
  input  nR4015,
  input  DMCINT,
  output nLFO1,
  output nLFO2,
  output D6_State,
  output INT
);

  wire _0, _0_t, _1, _1_t, _2, _2_t, _3, _3_t, _4, _4_t, _5, _5_t, _6, _6_t, _7, _7_t, _8, _8_t, _9, _9_t,
       _10, _10_t, _11, _11_t, _12, _12_t, _13, _13_t, _14, _14_t, and_1_out, and_2_out, d_ff_1_qn, d_ff_2_q,
       d_ff_3_qn, d_ff_4_qn, d_ff_5_qn, d_ff_6_qn, d_ff_7_qn, d_ff_8_qn, d_ff_9_qn, d_ff_10_qn, d_ff_11_qn,
       d_ff_12_qn, d_ff_13_qn, d_ff_14_qn, d_ff_15_qn, d_ff_16_qn, d_ff_17_qn, d_latch_1_not_q, d_latch_1_q,
       d_latch_2_not_q, d_latch_2_q, d_latch_3_q, Nor0_out, Nor1_out, Nor2_out, Nor3_out, Nor4_out, Nor5_out,
       nor_1_out, nor_2_out, nor_3_out, nor_4_out, nor_5_out, nor_6_out, nor_7_out, nor_8_out, nor_9_out,
       nor_10_out, nor_11_out, nor_12_out, nor_13_out, nor_14_out, nor_15_out, nor_16_out, nor_17_out,
       not_1_out, not_2_out, not_3_out;

  nor nor_1 (nor_1_out, ACLK, d_latch_1_q);
  nor nor_2 (nor_2_out, nor_1_out, nor_3_out);
  nor nor_3 (nor_3_out, nor_2_out, W4017, Res);
  nor nor_4 (nor_4_out, Nor5_out, _14_t, _13_t);
  and and_1 (and_1_out, _14_t, _13_t);
  nor Nor5 (Nor5_out, _0_t, _1_t, _2_t, _3_t, _4_t, _5_t, _6_t, _7_t, _8_t, _9_t, _10_t, _11_t, _12_t, _13_t, _14_t);
  D_latch d_latch_1 (.EN(nACLK), .D(nor_3_out), .Q(d_latch_1_q), .NOT_Q(d_latch_1_not_q));
  D_latch d_latch_2 (.EN(nACLK), .D(d_ff_1_qn), .Q(d_latch_2_q), .NOT_Q(d_latch_2_not_q));
  D_Flip_Flop #(.trigger("high")) d_ff_1 (
    .clk(not_1_out), .D(D7), .Qn(d_ff_1_qn), .en(W4017));  // open: Q, preset, reset
  not not_1 (not_1_out, nACLK);
  D_Flip_Flop #(.trigger("high")) d_ff_2 (
    .clk(not_1_out), .D(D6), .Q(d_ff_2_q), .en(W4017));  // open: Qn, preset, reset
  nor nor_5 (nor_5_out, nor_4_out, and_1_out);
  nor nor_6 (nor_6_out, not_2_out, ACLK);
  nor nor_7 (nor_7_out, d_latch_1_q, d_latch_2_q);
  nor nor_8 (nor_8_out, ACLK, nor_9_out);
  not not_2 (not_2_out, nor_9_out);
  nor nor_9 (nor_9_out, d_latch_1_not_q, Nor4_out, Nor3_out);
  D_Flip_Flop #(.trigger("high")) d_ff_3 (
    .clk(nor_6_out), .D(nor_5_out), .Qn(d_ff_3_qn), .preset(nor_8_out));  // open: Q, en, reset
  D_Flip_Flop #(.trigger("high")) d_ff_4 (
    .clk(nor_6_out), .D(_0_t), .Qn(d_ff_4_qn), .preset(nor_8_out));  // open: Q, en, reset
  D_Flip_Flop #(.trigger("high")) d_ff_5 (
    .clk(nor_6_out), .D(_1_t), .Qn(d_ff_5_qn), .preset(nor_8_out));  // open: Q, en, reset
  D_Flip_Flop #(.trigger("high")) d_ff_6 (
    .clk(nor_6_out), .D(_2_t), .Qn(d_ff_6_qn), .preset(nor_8_out));  // open: Q, en, reset
  D_Flip_Flop #(.trigger("high")) d_ff_7 (
    .clk(nor_6_out), .D(_3_t), .Qn(d_ff_7_qn), .preset(nor_8_out));  // open: Q, en, reset
  D_Flip_Flop #(.trigger("high")) d_ff_8 (
    .clk(nor_6_out), .D(_4_t), .Qn(d_ff_8_qn), .preset(nor_8_out));  // open: Q, en, reset
  D_Flip_Flop #(.trigger("high")) d_ff_9 (
    .clk(nor_6_out), .D(_5_t), .Qn(d_ff_9_qn), .preset(nor_8_out));  // open: Q, en, reset
  D_Flip_Flop #(.trigger("high")) d_ff_10 (
    .clk(nor_6_out), .D(_6_t), .Qn(d_ff_10_qn), .preset(nor_8_out));  // open: Q, en, reset
  D_Flip_Flop #(.trigger("high")) d_ff_11 (
    .clk(nor_6_out), .D(_7_t), .Qn(d_ff_11_qn), .preset(nor_8_out));  // open: Q, en, reset
  D_Flip_Flop #(.trigger("high")) d_ff_12 (
    .clk(nor_6_out), .D(_8_t), .Qn(d_ff_12_qn), .preset(nor_8_out));  // open: Q, en, reset
  D_Flip_Flop #(.trigger("high")) d_ff_13 (
    .clk(nor_6_out), .D(_9_t), .Qn(d_ff_13_qn), .preset(nor_8_out));  // open: Q, en, reset
  D_Flip_Flop #(.trigger("high")) d_ff_14 (
    .clk(nor_6_out), .D(_10_t), .Qn(d_ff_14_qn), .preset(nor_8_out));  // open: Q, en, reset
  D_Flip_Flop #(.trigger("high")) d_ff_15 (
    .clk(nor_6_out), .D(_11_t), .Qn(d_ff_15_qn), .preset(nor_8_out));  // open: Q, en, reset
  D_Flip_Flop #(.trigger("high")) d_ff_16 (
    .clk(nor_6_out), .D(_12_t), .Qn(d_ff_16_qn), .preset(nor_8_out));  // open: Q, en, reset
  D_Flip_Flop #(.trigger("high")) d_ff_17 (
    .clk(nor_6_out), .D(_13_t), .Qn(d_ff_17_qn), .preset(nor_8_out));  // open: Q, en, reset
  D_Flip_Flop #(.trigger("high")) d_ff_18 (.clk(nACLK), .D(d_ff_3_qn), .Q(_0), .Qn(_0_t));  // open: preset, en, reset
  D_Flip_Flop #(.trigger("high")) d_ff_19 (.clk(nACLK), .D(d_ff_4_qn), .Q(_1), .Qn(_1_t));  // open: preset, en, reset
  D_Flip_Flop #(.trigger("high")) d_ff_20 (.clk(nACLK), .D(d_ff_5_qn), .Q(_2), .Qn(_2_t));  // open: preset, en, reset
  D_Flip_Flop #(.trigger("high")) d_ff_21 (.clk(nACLK), .D(d_ff_6_qn), .Q(_3), .Qn(_3_t));  // open: preset, en, reset
  D_Flip_Flop #(.trigger("high")) d_ff_22 (.clk(nACLK), .D(d_ff_7_qn), .Q(_4), .Qn(_4_t));  // open: preset, en, reset
  D_Flip_Flop #(.trigger("high")) d_ff_23 (.clk(nACLK), .D(d_ff_8_qn), .Q(_5), .Qn(_5_t));  // open: preset, en, reset
  D_Flip_Flop #(.trigger("high")) d_ff_24 (.clk(nACLK), .D(d_ff_9_qn), .Q(_6), .Qn(_6_t));  // open: preset, en, reset
  D_Flip_Flop #(.trigger("high")) d_ff_25 (.clk(nACLK), .D(d_ff_10_qn), .Q(_7), .Qn(_7_t));  // open: preset, en, reset
  D_Flip_Flop #(.trigger("high")) d_ff_26 (.clk(nACLK), .D(d_ff_11_qn), .Q(_8), .Qn(_8_t));  // open: preset, en, reset
  D_Flip_Flop #(.trigger("high")) d_ff_27 (.clk(nACLK), .D(d_ff_12_qn), .Q(_9), .Qn(_9_t));  // open: preset, en, reset
  D_Flip_Flop #(.trigger("high")) d_ff_28 (
    .clk(nACLK), .D(d_ff_13_qn), .Q(_10), .Qn(_10_t));  // open: preset, en, reset
  D_Flip_Flop #(.trigger("high")) d_ff_29 (
    .clk(nACLK), .D(d_ff_14_qn), .Q(_11), .Qn(_11_t));  // open: preset, en, reset
  D_Flip_Flop #(.trigger("high")) d_ff_30 (
    .clk(nACLK), .D(d_ff_15_qn), .Q(_12), .Qn(_12_t));  // open: preset, en, reset
  D_Flip_Flop #(.trigger("high")) d_ff_31 (
    .clk(nACLK), .D(d_ff_16_qn), .Q(_13), .Qn(_13_t));  // open: preset, en, reset
  D_Flip_Flop #(.trigger("high")) d_ff_32 (
    .clk(nACLK), .D(d_ff_17_qn), .Q(_14), .Qn(_14_t));  // open: preset, en, reset
  and and_2 (and_2_out, Nor3_out, d_ff_1_qn);
  nor nor_10 (nor_10_out, PHI1, nR4015);
  nor nor_11 (nor_11_out, and_2_out, nor_12_out);
  nor nor_12 (nor_12_out, nor_11_out, d_ff_2_q, Res, nor_10_out);
  D_latch d_latch_3 (.EN(nACLK), .D(nor_11_out), .Q(d_latch_3_q));  // open: NOT_Q
  nor Nor0 (Nor0_out, _0, _1_t, _2_t, _3_t, _4_t, _5, _6, _7_t, _8_t, _9_t, _10_t, _11_t, _12, _13_t, _14_t);
  nor Nor1 (Nor1_out, _0, _1, _2_t, _3_t, _4_t, _5_t, _6_t, _7_t, _8_t, _9, _10, _11_t, _12, _13, _14_t);
  nor Nor2 (Nor2_out, _0, _1, _2_t, _3_t, _4, _5_t, _6, _7, _8_t, _9_t, _10, _11, _12_t, _13, _14_t);
  nor Nor3 (Nor3_out, _0, _1, _2, _3, _4, _5_t, _6_t, _7_t, _8_t, _9, _10_t, _11, _12_t, _13_t, _14_t, d_latch_2_not_q);
  nor Nor4 (Nor4_out, _0, _1_t, _2, _3_t, _4_t, _5_t, _6_t, _7, _8, _9_t, _10_t, _11_t, _12, _13, _14);
  assign D6_State = not_3_out ? ~d_latch_3_q : 1'bz;  // Controlled_Inverter controlled_inverter_1
  not not_3 (not_3_out, nR4015);
  nor nor_13 (nor_13_out, Nor0_out, Nor2_out, Nor1_out, Nor3_out, Nor4_out, nor_7_out);
  nor nor_14 (nor_14_out, Nor1_out, Nor3_out, Nor4_out, nor_7_out);
  nor nor_15 (nor_15_out, nor_12_out, DMCINT);
  not not_4 (INT, nor_15_out);
  not not_5 (nLFO1, nor_16_out);
  nor nor_16 (nor_16_out, ACLK, nor_13_out);
  not not_6 (nLFO2, nor_17_out);
  nor nor_17 (nor_17_out, ACLK, nor_14_out);

  // Notes on the sheet:
  //   Nor5=3728  X1
  //   Nor4=7456  X2
  //   Nor3=11184  X3
  //   Nor2=14914  X4
  //   Nor1=18640  X5
  //   R
  //   RS2
  //   S
  //   Nor0=16384  CARRY COUNT
  //   NOR6
  //   Q
  //   NORFF1
  //   CLEAR LFO
  //   NORFF2
  //   /Q
  //   NOR 5 NTSC = NOR5 PAL
  //   DL3
  //   DL6
  //   MD_Latch
  //   MODE  FLAG
  //   RESET INT FLAG
  //   Z1
  //   Z2
  //   4 OR 5 STEP
  //   IRQ DISABLE
  //   0
  //   1
  //   2
  //   3
  //   4
  //   5
  //   6
  //   7
  //   8
  //   9
  //   10
  //   11
  //   12
  //   13
  //   14
  //   S
  //   R
  //   INT FLAG
  //   NORFF2
  //   RS1
  //   NORFF1
  //   /Q
  //   Q
  //   INT STATUS
  //   0
  //   1
  //   NTSC   NOR  CONFIGURATION
  //   2
  //   3
  //   4
  //   NOR 5 NTSC = NOR5 PAL
  //   0
  //   1
  //   PAL   NOR  CONFIGURATION
  //   2
  //   3
  //   4
endmodule

module ACLK (
  input  PHI0,
  input  RES,
  output PHI1,
  output PHI2,
  output ACLK,
  output nACLK
);

  wire d_ff_1_qn, d_ff_2_qn, nor_1_out, nor_2_out, not_2_out;

  not not_1 (PHI1, PHI0);
  D_Flip_Flop #(.trigger("high")) d_ff_1 (.clk(PHI1), .D(nor_1_out), .Qn(d_ff_1_qn));  // open: Q, preset, en, reset
  not not_2 (not_2_out, PHI1);
  D_Flip_Flop #(.trigger("high")) d_ff_2 (.clk(PHI0), .D(d_ff_1_qn), .Qn(d_ff_2_qn));  // open: Q, preset, en, reset
  nor nor_1 (nor_1_out, RES, d_ff_2_qn);
  not not_3 (ACLK, nor_2_out);
  nor nor_2 (nor_2_out, nor_1_out, not_2_out);
  nor nor_3 (nACLK, not_2_out, d_ff_2_qn);

  assign PHI2 = PHI0;

  // Notes on the sheet:
  //   /ACLK2
  //   PHI1
  //   PHI2
  //   ACLK
  //   /ACLK
  //   DL1
  //   INV1
  //   DL2
  //   NOR1
  //   NOR2
  //   NOR3
endmodule

// CLK DIVIDER
module CLK_DIVIDER (
  input  nCLK,
  input  PHI2_CPU,
  output PHI0_CPU,
  output nM2
);

  wire d_latch_1_not_q, d_latch_2_not_q, d_latch_3_not_q, d_latch_4_not_q, d_latch_5_not_q, d_latch_6_not_q,
       d_latch_7_not_q, d_latch_8_not_q, d_latch_10_not_q, d_latch_11_q, d_latch_12_q, d_latch_13_q,
       d_latch_14_q, d_latch_15_q, d_latch_16_q, demultiplexer_1_out0, demultiplexer_1_out1, nor_1_out,
       nor_2_out, nor_3_out, nor_5_out, nor_6_out, nor_7_out, nor_8_out, nor_9_out, nor_10_out, not_1_out,
       not_2_out, or_1_out;

  not not_1 (not_1_out, nCLK);
  not not_2 (not_2_out, not_1_out);
  nor nor_1 (nor_1_out, not_1_out, nor_2_out);
  nor nor_2 (nor_2_out, nor_1_out, not_2_out);
  D_latch d_latch_1 (.EN(nor_2_out), .D(d_latch_10_not_q), .NOT_Q(d_latch_1_not_q));  // open: Q
  D_latch d_latch_2 (.EN(nor_2_out), .D(nor_5_out), .NOT_Q(d_latch_2_not_q));  // open: Q
  D_latch d_latch_3 (.EN(nor_2_out), .D(nor_6_out), .NOT_Q(d_latch_3_not_q));  // open: Q
  D_latch d_latch_4 (.EN(nor_2_out), .D(nor_7_out), .NOT_Q(d_latch_4_not_q));  // open: Q
  D_latch d_latch_5 (.EN(nor_2_out), .D(nor_8_out), .NOT_Q(d_latch_5_not_q));  // open: Q
  D_latch d_latch_6 (.EN(nor_2_out), .D(or_1_out), .NOT_Q(d_latch_6_not_q));  // open: Q
  D_latch d_latch_7 (.EN(nor_2_out), .D(nor_10_out), .NOT_Q(d_latch_7_not_q));  // open: Q
  D_latch d_latch_8 (.EN(nor_2_out), .D(demultiplexer_1_out1), .NOT_Q(d_latch_8_not_q));  // open: Q
  D_latch d_latch_9 (.EN(nor_1_out), .D(d_latch_1_not_q), .Q(PHI0_CPU));  // open: NOT_Q
  D_latch d_latch_10 (.EN(nor_1_out), .D(d_latch_2_not_q), .NOT_Q(d_latch_10_not_q));  // open: Q
  D_latch d_latch_11 (.EN(nor_1_out), .D(d_latch_3_not_q), .Q(d_latch_11_q));  // open: NOT_Q
  D_latch d_latch_12 (.EN(nor_1_out), .D(d_latch_4_not_q), .Q(d_latch_12_q));  // open: NOT_Q
  D_latch d_latch_13 (.EN(nor_1_out), .D(d_latch_5_not_q), .Q(d_latch_13_q));  // open: NOT_Q
  D_latch d_latch_14 (.EN(nor_1_out), .D(d_latch_6_not_q), .Q(d_latch_14_q));  // open: NOT_Q
  D_latch d_latch_15 (.EN(nor_1_out), .D(d_latch_7_not_q), .Q(d_latch_15_q));  // open: NOT_Q
  D_latch d_latch_16 (.EN(nor_1_out), .D(d_latch_8_not_q), .Q(d_latch_16_q));  // open: NOT_Q
  nor nor_3 (nor_3_out, PHI0_CPU, d_latch_10_not_q);
  nor nor_4 (nM2, d_latch_2_not_q, PHI2_CPU);
  nor nor_5 (nor_5_out, nor_3_out, d_latch_11_q);
  nor nor_6 (nor_6_out, nor_3_out, d_latch_12_q);
  nor nor_7 (nor_7_out, nor_3_out, d_latch_13_q);
  nor nor_8 (nor_8_out, nor_3_out, d_latch_14_q);
  nor nor_9 (nor_9_out, nor_3_out, d_latch_15_q);
  nor nor_10 (nor_10_out, nor_3_out, d_latch_16_q);
  or or_1 (or_1_out, demultiplexer_1_out0, nor_9_out);
  Demultiplexer #(.disabled(0), .enable("false")) demultiplexer_1 (
    .out0(demultiplexer_1_out0), .out1(demultiplexer_1_out1), .in(PHI0_CPU), .sel(1'b0));

  // Notes on the sheet:
  //   INV2
  //   NOR1
  //   NOR2
  //   0 NTSC
  //   1 PAL
  //   #CLK
  //   PHI0 NTSC
  //   PHI0 PAL
endmodule

// REGISTER SELECT
module REGISTER_SELECT (
  input  PHI1,
  input  R_W,
  input  A15,
  input  A14,
  input  A13,
  input  A12,
  input  A11,
  input  A10,
  input  A9,
  input  A8,
  input  A7,
  input  A6,
  input  A5,
  input  A4,
  input  A3,
  input  A2,
  input  A1,
  input  A0,
  input  DBG,
  output W4000,
  output W4001,
  output W4002,
  output W4003,
  output W4004,
  output W4005,
  output W4006,
  output W4007,
  output W4008,
  output W400A,
  output W400B,
  output W400C,
  output W400E,
  output W400F,
  output W4010,
  output W4011,
  output W4012,
  output W4013,
  output W4014,
  output W4015,
  output W4016,
  output W4017,
  output W401A,
  output nR4015,
  output nR4016,
  output nR4017,
  output nR4018,
  output nR4019,
  output nR401A,
  output nDBGRD
);

  wire and_1_out, decoder_1_out26, decoder_2_out21, decoder_2_out22, decoder_2_out23, decoder_2_out24,
       decoder_2_out25, decoder_2_out26, demultiplexer_1_out0, demultiplexer_1_out1, nor_1_out, not_1_out,
       not_2_out;

  not not_1 (not_1_out, A14);
  nor nor_1 (nor_1_out, A15, not_1_out, A13, A12, A11, A10, A9, A8, A7, A6, A5);
  Demultiplexer #(.enable("false")) demultiplexer_1 (
    .out0(demultiplexer_1_out0), .out1(demultiplexer_1_out1), .in(nor_1_out), .sel(R_W));
  and and_1 (and_1_out, ~PHI1, demultiplexer_1_out0);  // AND_Gate
  Decoder #(.select(5), .disabled(0)) decoder_1 (
    .out0(W4000), .out1(W4001), .out2(W4002), .out3(W4003), .out4(W4004), .out5(W4005), .out6(W4006),
    .out7(W4007), .out8(W4008), .out10(W400A), .out11(W400B), .out12(W400C), .out14(W400E), .out15(W400F),
    .out16(W4010), .out17(W4011), .out18(W4012), .out19(W4013), .out20(W4014), .out21(W4015), .out22(W4016),
    .out23(W4017), .out26(decoder_1_out26), .sel({A4, A3, A2, A1, A0}), .en(and_1_out));  // open: out9, out13, out24, out25, out27, out28, out29, out30, out31
  Decoder #(.select(5), .disabled(0)) decoder_2 (
    .out21(decoder_2_out21), .out22(decoder_2_out22), .out23(decoder_2_out23), .out24(decoder_2_out24),
    .out25(decoder_2_out25), .out26(decoder_2_out26), .sel({A4, A3, A2, A1, A0}), .en(demultiplexer_1_out1));  // open: out0, out1, out2, out3, out4, out5, out6, out7, out8, out9, out10, out11, out12, out13, out14, out15, out16, out17, out18, out19, out20, out27, out28, out29, out30, out31
  not not_2 (not_2_out, demultiplexer_1_out1);
  and and_2 (W401A, decoder_1_out26, DBG);
  not not_3 (nR4015, decoder_2_out21);
  not not_4 (nR4016, decoder_2_out22);
  not not_5 (nR4017, decoder_2_out23);
  nand nand_1 (nR4018, decoder_2_out24, DBG);
  nand nand_2 (nR4019, decoder_2_out25, DBG);
  nand nand_3 (nR401A, decoder_2_out26, DBG);
  nand nand_4 (nDBGRD, DBG, not_2_out);

  // Notes on the sheet:
  //   REGWR
  //   Enable write ports
  //   REGRD
  //   Enable read ports
endmodule

// ENVELOPE GENERATOR
module ENVELOPE_GENERATOR (
  input  nACLK,
  input  RES,
  input  W400_0__4__C,
  input  D0,
  input  D1,
  input  D2,
  input  D3,
  input  D4,
  input  D5,
  input  W400_3__7__F,
  input  nLFO1,
  input  CH_IN,
  output [5:0] ENV,
  output V0,
  output V1,
  output V2,
  output V3,
  output nCH_LC
);

  wire _7_out, _8_out, _11_out, _12_out, _13_out, _14_out, _15_out, _16_out, _18_out, _19_out, d_ff_7_q,
       d_ff_7_qn, d_ff_8_q, d_ff_8_qn, d_ff_9_q, d_ff_9_qn, d_ff_10_q, d_ff_10_qn, d_ff_11_q, d_ff_11_qn,
       d_ff_12_q, d_ff_12_qn, d_ff_13_q, d_ff_13_qn, d_ff_14_q, d_ff_14_qn, d_ff_15_qn, d_ff_16_qn,
       d_ff_17_qn, d_ff_18_qn, d_ff_19_qn, d_ff_20_qn, d_ff_21_qn, d_ff_22_qn, d_latch_1_q, d_latch_2_not_q,
       d_latch_2_q, d_latch_3_q, d_latch_4_q, demultiplexer_1_out0, demultiplexer_1_out1,
       demultiplexer_2_out0, demultiplexer_2_out1, demultiplexer_3_out0, demultiplexer_3_out1,
       demultiplexer_4_out0, demultiplexer_4_out1, demultiplexer_5_out0, demultiplexer_5_out1,
       demultiplexer_6_out0, demultiplexer_6_out1, demultiplexer_7_out0, demultiplexer_7_out1,
       demultiplexer_8_out0, demultiplexer_8_out1, multiplexer_1_out, multiplexer_2_out, multiplexer_3_out,
       multiplexer_4_out, nor_1_out, nor_2_out, nor_3_out, nor_4_out, nor_5_out, nor_6_out, nor_7_out,
       nor_8_out, not_1_out, not_2_out, not_3_out, not_4_out, not_5_out, not_6_out, not_7_out, not_8_out,
       not_9_out, not_10_out, not_11_out, not_12_out, not_13_out, not_14_out, not_15_out, or_1_out, or_2_out,
       or_3_out, or_4_out, or_5_out, or_6_out, or_7_out, or_8_out, xor_1_out, xor_2_out, xor_3_out,
       xor_4_out, xor_5_out, xor_6_out, xor_7_out, xor_8_out;

  not not_1 (not_1_out, nACLK);
  D_Flip_Flop #(.trigger("high")) d_ff_1 (
    .clk(not_1_out), .D(D0), .Q(ENV[0]), .en(W400_0__4__C));  // open: Qn, preset, reset
  D_Flip_Flop #(.trigger("high")) d_ff_2 (
    .clk(not_1_out), .D(D1), .Q(ENV[1]), .en(W400_0__4__C));  // open: Qn, preset, reset
  D_Flip_Flop #(.trigger("high")) d_ff_3 (
    .clk(not_1_out), .D(D2), .Q(ENV[2]), .en(W400_0__4__C));  // open: Qn, preset, reset
  D_Flip_Flop #(.trigger("high")) d_ff_4 (
    .clk(not_1_out), .D(D3), .Q(ENV[3]), .en(W400_0__4__C));  // open: Qn, preset, reset
  D_Flip_Flop #(.trigger("high")) d_ff_5 (
    .clk(not_1_out), .D(D4), .Q(ENV[4]), .en(W400_0__4__C));  // open: Qn, preset, reset
  D_Flip_Flop #(.trigger("high")) d_ff_6 (
    .clk(not_1_out), .D(D5), .Q(ENV[5]), .Qn(nCH_LC), .en(W400_0__4__C));  // open: preset, reset
  Demultiplexer #(.enable("false")) demultiplexer_1 (
    .out0(demultiplexer_1_out0), .out1(demultiplexer_1_out1), .in(_16_out), .sel(ENV[0]));
  Demultiplexer #(.enable("false")) demultiplexer_2 (
    .out0(demultiplexer_2_out0), .out1(demultiplexer_2_out1), .in(_16_out), .sel(ENV[1]));
  Demultiplexer #(.enable("false")) demultiplexer_3 (
    .out0(demultiplexer_3_out0), .out1(demultiplexer_3_out1), .in(_16_out), .sel(ENV[2]));
  Demultiplexer #(.enable("false")) demultiplexer_4 (
    .out0(demultiplexer_4_out0), .out1(demultiplexer_4_out1), .in(_16_out), .sel(ENV[3]));
  Demultiplexer #(.enable("false")) demultiplexer_5 (
    .out0(demultiplexer_5_out0), .out1(demultiplexer_5_out1), .in(_8_out), .sel(_12_out));
  Demultiplexer #(.enable("false")) demultiplexer_6 (
    .out0(demultiplexer_6_out0), .out1(demultiplexer_6_out1), .in(_8_out), .sel(_12_out));
  Demultiplexer #(.enable("false")) demultiplexer_7 (
    .out0(demultiplexer_7_out0), .out1(demultiplexer_7_out1), .in(_8_out), .sel(_12_out));
  Demultiplexer #(.enable("false")) demultiplexer_8 (
    .out0(demultiplexer_8_out0), .out1(demultiplexer_8_out1), .in(_8_out), .sel(_12_out));
  or or_1 (or_1_out, RES, demultiplexer_1_out0);
  or or_2 (or_2_out, RES, demultiplexer_2_out0);
  or or_3 (or_3_out, RES, demultiplexer_3_out0);
  or or_4 (or_4_out, RES, demultiplexer_4_out0);
  or or_5 (or_5_out, RES, demultiplexer_5_out0);
  or or_6 (or_6_out, RES, demultiplexer_6_out0);
  or or_7 (or_7_out, RES, demultiplexer_7_out0);
  or or_8 (or_8_out, RES, demultiplexer_8_out0);
  D_Flip_Flop #(.trigger("high")) d_ff_7 (
    .clk(_18_out), .D(d_ff_15_qn), .Q(d_ff_7_q), .Qn(d_ff_7_qn), .preset(demultiplexer_1_out1),
    .reset(or_1_out));  // open: en
  D_Flip_Flop #(.trigger("high")) d_ff_8 (
    .clk(_18_out), .D(d_ff_16_qn), .Q(d_ff_8_q), .Qn(d_ff_8_qn), .preset(demultiplexer_2_out1),
    .reset(or_2_out));  // open: en
  D_Flip_Flop #(.trigger("high")) d_ff_9 (
    .clk(_18_out), .D(d_ff_17_qn), .Q(d_ff_9_q), .Qn(d_ff_9_qn), .preset(demultiplexer_3_out1),
    .reset(or_3_out));  // open: en
  D_Flip_Flop #(.trigger("high")) d_ff_10 (
    .clk(_18_out), .D(d_ff_18_qn), .Q(d_ff_10_q), .Qn(d_ff_10_qn), .preset(demultiplexer_4_out1),
    .reset(or_4_out));  // open: en
  D_Flip_Flop #(.trigger("high")) d_ff_11 (
    .clk(_7_out), .D(d_ff_19_qn), .Q(d_ff_11_q), .Qn(d_ff_11_qn), .preset(demultiplexer_5_out1),
    .reset(or_5_out));  // open: en
  D_Flip_Flop #(.trigger("high")) d_ff_12 (
    .clk(_7_out), .D(d_ff_20_qn), .Q(d_ff_12_q), .Qn(d_ff_12_qn), .preset(demultiplexer_6_out1),
    .reset(or_6_out));  // open: en
  D_Flip_Flop #(.trigger("high")) d_ff_13 (
    .clk(_7_out), .D(d_ff_21_qn), .Q(d_ff_13_q), .Qn(d_ff_13_qn), .preset(demultiplexer_7_out1),
    .reset(or_7_out));  // open: en
  D_Flip_Flop #(.trigger("high")) d_ff_14 (
    .clk(_7_out), .D(d_ff_22_qn), .Q(d_ff_14_q), .Qn(d_ff_14_qn), .preset(demultiplexer_8_out1),
    .reset(or_8_out));  // open: en
  not not_2 (not_2_out, 1'b1);
  not not_3 (not_3_out, nor_1_out);
  not not_4 (not_4_out, nor_2_out);
  not not_5 (not_5_out, nor_3_out);
  nor _15 (_15_out, _19_out, _14_out);
  nor _14 (_14_out, _15_out, W400_3__7__F);
  nor _13 (_13_out, nor_4_out, _15_out);
  not not_6 (not_6_out, 1'b1);
  not not_7 (not_7_out, nor_5_out);
  not not_8 (not_8_out, nor_6_out);
  not not_9 (not_9_out, nor_7_out);
  xor xor_1 (xor_1_out, 1'b1, d_ff_7_qn);
  nor nor_1 (nor_1_out, not_2_out, d_ff_7_q);
  xor xor_2 (xor_2_out, nor_1_out, d_ff_8_qn);
  nor nor_2 (nor_2_out, not_3_out, d_ff_8_q);
  xor xor_3 (xor_3_out, nor_2_out, d_ff_9_qn);
  nor nor_3 (nor_3_out, not_4_out, d_ff_9_q);
  xor xor_4 (xor_4_out, nor_3_out, d_ff_10_qn);
  nor nor_4 (nor_4_out, not_5_out, d_ff_10_q);
  D_latch d_latch_1 (.EN(nACLK), .D(_14_out), .Q(d_latch_1_q));  // open: NOT_Q
  D_latch d_latch_2 (.EN(nACLK), .D(_13_out), .Q(d_latch_2_q), .NOT_Q(d_latch_2_not_q));
  xor xor_5 (xor_5_out, 1'b1, d_ff_11_qn);
  nor nor_5 (nor_5_out, not_6_out, d_ff_11_q);
  xor xor_6 (xor_6_out, nor_5_out, d_ff_12_qn);
  nor nor_6 (nor_6_out, not_7_out, d_ff_12_q);
  xor xor_7 (xor_7_out, nor_6_out, d_ff_13_qn);
  nor nor_7 (nor_7_out, not_8_out, d_ff_13_q);
  xor xor_8 (xor_8_out, nor_7_out, d_ff_14_qn);
  nor nor_8 (nor_8_out, not_9_out, _15_out, d_ff_14_q);
  D_Flip_Flop #(.trigger("high")) d_ff_15 (.clk(nACLK), .D(xor_1_out), .Qn(d_ff_15_qn));  // open: Q, preset, en, reset
  D_Flip_Flop #(.trigger("high")) d_ff_16 (.clk(nACLK), .D(xor_2_out), .Qn(d_ff_16_qn));  // open: Q, preset, en, reset
  D_Flip_Flop #(.trigger("high")) d_ff_17 (.clk(nACLK), .D(xor_3_out), .Qn(d_ff_17_qn));  // open: Q, preset, en, reset
  D_Flip_Flop #(.trigger("high")) d_ff_18 (.clk(nACLK), .D(xor_4_out), .Qn(d_ff_18_qn));  // open: Q, preset, en, reset
  nor _19 (_19_out, d_latch_1_q, nLFO1);
  nor _16 (_16_out, nLFO1, d_latch_2_q);
  nor _18 (_18_out, d_latch_2_not_q, nLFO1);
  D_Flip_Flop #(.trigger("high")) d_ff_19 (.clk(nACLK), .D(xor_5_out), .Qn(d_ff_19_qn));  // open: Q, preset, en, reset
  D_Flip_Flop #(.trigger("high")) d_ff_20 (.clk(nACLK), .D(xor_6_out), .Qn(d_ff_20_qn));  // open: Q, preset, en, reset
  D_Flip_Flop #(.trigger("high")) d_ff_21 (.clk(nACLK), .D(xor_7_out), .Qn(d_ff_21_qn));  // open: Q, preset, en, reset
  D_Flip_Flop #(.trigger("high")) d_ff_22 (.clk(nACLK), .D(xor_8_out), .Qn(d_ff_22_qn));  // open: Q, preset, en, reset
  D_latch d_latch_3 (.EN(nACLK), .D(nor_8_out), .Q(d_latch_3_q));  // open: NOT_Q
  D_latch d_latch_4 (.EN(nACLK), .D(_15_out), .Q(d_latch_4_q));  // open: NOT_Q
  nand _12 (_12_out, d_latch_3_q, nCH_LC);
  nor _11 (_11_out, d_latch_3_q, d_latch_4_q);
  not not_10 (not_10_out, _11_out);
  not not_11 (not_11_out, _16_out);
  nor _7 (_7_out, not_10_out, not_11_out);
  nor _8 (_8_out, _11_out, not_11_out);
  not not_12 (not_12_out, multiplexer_1_out);
  Multiplexer #(.enable("false")) multiplexer_1 (.in0(d_ff_11_q), .in1(ENV[0]), .out(multiplexer_1_out), .sel(ENV[4]));
  not not_13 (not_13_out, multiplexer_2_out);
  Multiplexer #(.enable("false")) multiplexer_2 (.in0(d_ff_12_q), .in1(ENV[1]), .out(multiplexer_2_out), .sel(ENV[4]));
  not not_14 (not_14_out, multiplexer_3_out);
  Multiplexer #(.enable("false")) multiplexer_3 (.in0(d_ff_13_q), .in1(ENV[2]), .out(multiplexer_3_out), .sel(ENV[4]));
  not not_15 (not_15_out, multiplexer_4_out);
  Multiplexer #(.enable("false")) multiplexer_4 (.in0(d_ff_14_q), .in1(ENV[3]), .out(multiplexer_4_out), .sel(ENV[4]));
  nor nor_9 (V0, not_12_out, CH_IN);
  nor nor_10 (V1, not_13_out, CH_IN);
  nor nor_11 (V2, not_14_out, CH_IN);
  nor nor_12 (V3, not_15_out, CH_IN);

  // Notes on the sheet:
  //   W4000(SQR A)
  //   W4004 (SQR B)
  //   W400C (NOISE)
  //   W4003 (SQR A)
  //   W4007 (SQR B)
  //   W400F (NOISE)
  //   ENVDIS
  //   #SQA(B)(NOISE)/LC
  //   RELOAD
  //   ENVELOPE DECAY DOWN COUNTER
  //   R
  //   RS1
  //   S
  //   ENVELOPE DOWN COUNTER
  //   Q
  //   /Q
  //   DL6
  //   DL10
  //   The signal names are shown for the noise channel. For square channels A and B, the designation changes instead of N to A or B, respectively
  //   RLOAD
  //   RSTEP
  //   DL7
  //   DL9
  //   VOL0
  //   VOL1
  //   VOL2
  //   VOL3
  //   ENV0
  //   ENV1
  //   ENV2
  //   ENV3
  //   RLOAD
  //   EIN
  //   10
  //   9
  //   ENVDIS
  //   ESTEP
  //   ERES
endmodule

// SQUARE CHANNEL 0
module SQUARE_CHANNEL_0 (
  input  ACLK,
  input  nACLK,
  input  W4003,
  input  W4000,
  input  W4002,
  input  D0,
  input  D1,
  input  D2,
  input  D3,
  input  D4,
  input  D5,
  input  D6,
  input  D7,
  input  LOCK,
  input  W4001,
  input  nLFO2,
  input  RES,
  input  NOSQA,
  input  nLFO1,
  output [10:0] SQA_F,
  output [1:0] SQA_DUTY,
  output [5:0] SQA_ENV,
  output SQA0,
  output SQA1,
  output SQ2,
  output [7:0] SWEEP_REG,
  output SQA3,
  output nSQA_LC
);

  wire d_latch_1_q, nor_1_out, nor_2_out, nor_3_out, not_1_out, not_2_out, not_3_out, square_adder_1_ncout,
       square_barrel_shifter_1_s0, square_barrel_shifter_1_s1, square_barrel_shifter_1_s2,
       square_barrel_shifter_1_s3, square_barrel_shifter_1_s4, square_barrel_shifter_1_s5,
       square_barrel_shifter_1_s6, square_barrel_shifter_1_s7, square_barrel_shifter_1_s8,
       square_barrel_shifter_1_s9, square_barrel_shifter_1_s10, square_duty_down_counter_1_sqout,
       square_frequency_down_counter_1_fload, square_frequency_down_counter_1_fqout, square_register_1_mu0,
       square_register_1_mu1, square_register_1_mu2, square_register_1_mu3, square_register_1_mu4,
       square_register_1_mu5, square_register_1_mu6, square_register_1_mu7, square_register_1_mu8,
       square_register_1_mu9, square_register_1_mu10, square_sweep_control_1_d_i,
       square_sweep_control_1_do_sweep, square_sweep_control_1_sw_ovf;
  wire [2:0] square_sweep_control_1_sr0;
  wire [10:0] square_adder_1_nsum0;

  not not_1 (not_1_out, ACLK);
  SQUARE_SWEEP_CONTROL square_sweep_control_1 (
    .nACLK(nACLK), .W400x(W4001), .D0(D0), .D1(D1), .D2(D2), .D3(D3), .D4(D4), .D5(D5), .D6(D6), .D7(D7),
    .nLFO2(nLFO2), .NOSQA(NOSQA), .nCOUT(square_adder_1_ncout), .SW_UVF(nor_3_out), .RES(RES),
    .SR0(square_sweep_control_1_sr0[0]), .SR1(square_sweep_control_1_sr0[1]),
    .SR2(square_sweep_control_1_sr0[2]), .D_I(square_sweep_control_1_d_i),
    .DO_SWEEP(square_sweep_control_1_do_sweep), .SW_OVF(square_sweep_control_1_sw_ovf), .SWEEP_REG(SWEEP_REG));
  not not_2 (not_2_out, square_sweep_control_1_d_i);
  SQUARE_REGISTER square_register_1 (
    .nACLK(nACLK), .nACLK3(not_1_out), .W4002(W4002), .W4003(W4003), .D0(D0), .D1(D1), .D2(D2), .D3(D3),
    .D4(D4), .D5(D5), .D6(D6), .D7(D7), .D_I(square_sweep_control_1_d_i), .F0(SQA_F[0]),
    .MU0(square_register_1_mu0), .nSum0(square_adder_1_nsum0[0]), .F1(SQA_F[1]), .MU1(square_register_1_mu1),
    .nSum1(square_adder_1_nsum0[1]), .F2(SQA_F[2]), .MU2(square_register_1_mu2),
    .nSum2(square_adder_1_nsum0[2]), .F3(SQA_F[3]), .MU3(square_register_1_mu3),
    .nSum3(square_adder_1_nsum0[3]), .F4(SQA_F[4]), .MU4(square_register_1_mu4),
    .nSum4(square_adder_1_nsum0[4]), .F5(SQA_F[5]), .MU5(square_register_1_mu5),
    .nSum5(square_adder_1_nsum0[5]), .F6(SQA_F[6]), .MU6(square_register_1_mu6),
    .nSum6(square_adder_1_nsum0[6]), .F7(SQA_F[7]), .MU7(square_register_1_mu7),
    .nSum7(square_adder_1_nsum0[7]), .F8(SQA_F[8]), .MU8(square_register_1_mu8),
    .nSum8(square_adder_1_nsum0[8]), .F9(SQA_F[9]), .MU9(square_register_1_mu9),
    .nSum9(square_adder_1_nsum0[9]), .F10(SQA_F[10]), .MU10(square_register_1_mu10),
    .DO_SWEEP(square_sweep_control_1_do_sweep), .nSum10(square_adder_1_nsum0[10]));
  SQUARE_BARREL_SHIFTER square_barrel_shifter_1 (
    .MUI0(square_register_1_mu0), .MUI1(square_register_1_mu1), .MUI2(square_register_1_mu2),
    .MUI3(square_register_1_mu3), .MUI4(square_register_1_mu4), .MUI5(square_register_1_mu5),
    .MUI6(square_register_1_mu6), .MUI7(square_register_1_mu7), .MUI8(square_register_1_mu8),
    .MUI9(square_register_1_mu9), .MUI10(square_register_1_mu10), .Dec_Inc(square_sweep_control_1_d_i),
    .SR0(square_sweep_control_1_sr0[0]), .SR1(square_sweep_control_1_sr0[1]),
    .SR2(square_sweep_control_1_sr0[2]), .S0(square_barrel_shifter_1_s0), .S1(square_barrel_shifter_1_s1),
    .S2(square_barrel_shifter_1_s2), .S3(square_barrel_shifter_1_s3), .S4(square_barrel_shifter_1_s4),
    .S5(square_barrel_shifter_1_s5), .S6(square_barrel_shifter_1_s6), .S7(square_barrel_shifter_1_s7),
    .S8(square_barrel_shifter_1_s8), .S9(square_barrel_shifter_1_s9), .S10(square_barrel_shifter_1_s10));
  not not_3 (not_3_out, square_duty_down_counter_1_sqout);
  SQUARE_ADDER square_adder_1 (
    .nCIN(1'b1), .FX0(SQA_F[0]), .nSum0(square_adder_1_nsum0[0]), .SX0(square_barrel_shifter_1_s0),
    .FX1(SQA_F[1]), .nSum1(square_adder_1_nsum0[1]), .SX1(square_barrel_shifter_1_s1), .FX2(SQA_F[2]),
    .nSum2(square_adder_1_nsum0[2]), .SX2(square_barrel_shifter_1_s2), .FX3(SQA_F[3]),
    .nSum3(square_adder_1_nsum0[3]), .SX3(square_barrel_shifter_1_s3), .FX4(SQA_F[4]),
    .nSum4(square_adder_1_nsum0[4]), .SX4(square_barrel_shifter_1_s4), .FX5(SQA_F[5]),
    .nSum5(square_adder_1_nsum0[5]), .SX5(square_barrel_shifter_1_s5), .FX6(SQA_F[6]),
    .nSum6(square_adder_1_nsum0[6]), .SX6(square_barrel_shifter_1_s6), .FX7(SQA_F[7]),
    .nSum7(square_adder_1_nsum0[7]), .SX7(square_barrel_shifter_1_s7), .FX8(SQA_F[8]),
    .nSum8(square_adder_1_nsum0[8]), .SX8(square_barrel_shifter_1_s8), .FX9(SQA_F[9]),
    .nSum9(square_adder_1_nsum0[9]), .SX9(square_barrel_shifter_1_s9), .nCOUT(square_adder_1_ncout),
    .FX10(SQA_F[10]), .SX10(square_barrel_shifter_1_s10), .nSum10(square_adder_1_nsum0[10]));
  nor nor_1 (nor_1_out, nor_3_out, not_3_out, square_sweep_control_1_sw_ovf, NOSQA);
  D_latch d_latch_1 (.EN(nACLK), .D(nor_1_out), .Q(d_latch_1_q));  // open: NOT_Q
  nor nor_2 (nor_2_out, d_latch_1_q, LOCK);
  nor nor_3 (nor_3_out, SQA_F[2], SQA_F[3], SQA_F[4], SQA_F[5], SQA_F[6], SQA_F[7], SQA_F[8], SQA_F[9], SQA_F[10]);
  SQUARE_FREQUENCY_DOWN_COUNTER square_frequency_down_counter_1 (
    .nACLK(nACLK), .ACLK(ACLK), .RES(RES), .PL0(SQA_F[0]), .PL1(SQA_F[1]), .PL2(SQA_F[2]), .PL3(SQA_F[3]),
    .PL4(SQA_F[4]), .PL5(SQA_F[5]), .PL6(SQA_F[6]), .PL7(SQA_F[7]), .PL8(SQA_F[8]), .PL9(SQA_F[9]),
    .PL10(SQA_F[10]), .FQOUT(square_frequency_down_counter_1_fqout),
    .FLOAD(square_frequency_down_counter_1_fload));
  SQUARE_DUTY_DOWN_COUNTER square_duty_down_counter_1 (
    .nACLK(nACLK), .FQOUT(square_frequency_down_counter_1_fqout), .RES(RES), .W4003(W4003),
    .FLOAD(square_frequency_down_counter_1_fload), .W4000(W4000), .D6(D6), .D7(D7),
    .SQOUT(square_duty_down_counter_1_sqout), .SQ_DUTY(SQA_DUTY));
  ENVELOPE_GENERATOR envelope_generator_1 (
    .nACLK(nACLK), .W400_0__4__C(W4000), .W400_3__7__F(W4003), .D0(D0), .D1(D1), .D2(D2), .D3(D3), .D4(D4),
    .D5(D5), .nLFO1(nLFO1), .RES(RES), .V0(SQA0), .V1(SQA1), .V2(SQ2), .V3(SQA3), .nCH_LC(nSQA_LC),
    .CH_IN(nor_2_out), .ENV(SQA_ENV));

  // Notes on the sheet:
  //   Connect to VCC for square0, connect to inverter for square1
  //   !!!
  //   INV5
  //   SW_UVF
endmodule

// SQUARE CHANNEL 1
module SQUARE_CHANNEL_1 (
  input  ACLK,
  input  nACLK,
  input  W4004,
  input  W4007,
  input  W4006,
  input  D0,
  input  D1,
  input  D2,
  input  D3,
  input  D4,
  input  D5,
  input  D6,
  input  D7,
  input  LOCK,
  input  W4005,
  input  nLFO2,
  input  RES,
  input  NOSQB,
  input  nLFO1,
  output [10:0] SQB_F,
  output [1:0] SQB_DUTY,
  output [5:0] SQB_ENV,
  output SQB0,
  output SQB1,
  output SQB2,
  output [7:0] SWEEP_REG,
  output SQB3,
  output nSQB_LC
);

  wire d_latch_1_q, nor_1_out, nor_2_out, nor_3_out, not_1_out, not_2_out, not_3_out, square_adder_1_ncout,
       square_barrel_shifter_1_s0, square_barrel_shifter_1_s1, square_barrel_shifter_1_s2,
       square_barrel_shifter_1_s3, square_barrel_shifter_1_s4, square_barrel_shifter_1_s5,
       square_barrel_shifter_1_s6, square_barrel_shifter_1_s7, square_barrel_shifter_1_s8,
       square_barrel_shifter_1_s9, square_barrel_shifter_1_s10, square_duty_down_counter_1_sqout,
       square_frequency_down_counter_1_fload, square_frequency_down_counter_1_fqout, square_register_1_mu0,
       square_register_1_mu1, square_register_1_mu2, square_register_1_mu3, square_register_1_mu4,
       square_register_1_mu5, square_register_1_mu6, square_register_1_mu7, square_register_1_mu8,
       square_register_1_mu9, square_register_1_mu10, square_sweep_control_1_d_i,
       square_sweep_control_1_do_sweep, square_sweep_control_1_sw_ovf;
  wire [2:0] square_sweep_control_1_sr0;
  wire [10:0] square_adder_1_nsum0;

  not not_1 (not_1_out, square_sweep_control_1_d_i);
  not not_2 (not_2_out, ACLK);
  SQUARE_SWEEP_CONTROL square_sweep_control_1 (
    .nACLK(nACLK), .W400x(W4005), .D0(D0), .D1(D1), .D2(D2), .D3(D3), .D4(D4), .D5(D5), .D6(D6), .D7(D7),
    .nLFO2(nLFO2), .NOSQA(NOSQB), .nCOUT(square_adder_1_ncout), .SW_UVF(nor_3_out), .RES(RES),
    .SR0(square_sweep_control_1_sr0[0]), .SR1(square_sweep_control_1_sr0[1]),
    .SR2(square_sweep_control_1_sr0[2]), .D_I(square_sweep_control_1_d_i),
    .DO_SWEEP(square_sweep_control_1_do_sweep), .SW_OVF(square_sweep_control_1_sw_ovf), .SWEEP_REG(SWEEP_REG));
  SQUARE_REGISTER square_register_1 (
    .nACLK(nACLK), .nACLK3(not_2_out), .W4002(W4006), .W4003(W4007), .D0(D0), .D1(D1), .D2(D2), .D3(D3),
    .D4(D4), .D5(D5), .D6(D6), .D7(D7), .D_I(square_sweep_control_1_d_i), .F0(SQB_F[0]),
    .MU0(square_register_1_mu0), .nSum0(square_adder_1_nsum0[0]), .F1(SQB_F[1]), .MU1(square_register_1_mu1),
    .nSum1(square_adder_1_nsum0[1]), .F2(SQB_F[2]), .MU2(square_register_1_mu2),
    .nSum2(square_adder_1_nsum0[2]), .F3(SQB_F[3]), .MU3(square_register_1_mu3),
    .nSum3(square_adder_1_nsum0[3]), .F4(SQB_F[4]), .MU4(square_register_1_mu4),
    .nSum4(square_adder_1_nsum0[4]), .F5(SQB_F[5]), .MU5(square_register_1_mu5),
    .nSum5(square_adder_1_nsum0[5]), .F6(SQB_F[6]), .MU6(square_register_1_mu6),
    .nSum6(square_adder_1_nsum0[6]), .F7(SQB_F[7]), .MU7(square_register_1_mu7),
    .nSum7(square_adder_1_nsum0[7]), .F8(SQB_F[8]), .MU8(square_register_1_mu8),
    .nSum8(square_adder_1_nsum0[8]), .F9(SQB_F[9]), .MU9(square_register_1_mu9),
    .nSum9(square_adder_1_nsum0[9]), .F10(SQB_F[10]), .MU10(square_register_1_mu10),
    .DO_SWEEP(square_sweep_control_1_do_sweep), .nSum10(square_adder_1_nsum0[10]));
  SQUARE_BARREL_SHIFTER square_barrel_shifter_1 (
    .MUI0(square_register_1_mu0), .MUI1(square_register_1_mu1), .MUI2(square_register_1_mu2),
    .MUI3(square_register_1_mu3), .MUI4(square_register_1_mu4), .MUI5(square_register_1_mu5),
    .MUI6(square_register_1_mu6), .MUI7(square_register_1_mu7), .MUI8(square_register_1_mu8),
    .MUI9(square_register_1_mu9), .MUI10(square_register_1_mu10), .Dec_Inc(square_sweep_control_1_d_i),
    .SR0(square_sweep_control_1_sr0[0]), .SR1(square_sweep_control_1_sr0[1]),
    .SR2(square_sweep_control_1_sr0[2]), .S0(square_barrel_shifter_1_s0), .S1(square_barrel_shifter_1_s1),
    .S2(square_barrel_shifter_1_s2), .S3(square_barrel_shifter_1_s3), .S4(square_barrel_shifter_1_s4),
    .S5(square_barrel_shifter_1_s5), .S6(square_barrel_shifter_1_s6), .S7(square_barrel_shifter_1_s7),
    .S8(square_barrel_shifter_1_s8), .S9(square_barrel_shifter_1_s9), .S10(square_barrel_shifter_1_s10));
  not not_3 (not_3_out, square_duty_down_counter_1_sqout);
  SQUARE_ADDER square_adder_1 (
    .nCIN(not_1_out), .FX0(SQB_F[0]), .nSum0(square_adder_1_nsum0[0]), .SX0(square_barrel_shifter_1_s0),
    .FX1(SQB_F[1]), .nSum1(square_adder_1_nsum0[1]), .SX1(square_barrel_shifter_1_s1), .FX2(SQB_F[2]),
    .nSum2(square_adder_1_nsum0[2]), .SX2(square_barrel_shifter_1_s2), .FX3(SQB_F[3]),
    .nSum3(square_adder_1_nsum0[3]), .SX3(square_barrel_shifter_1_s3), .FX4(SQB_F[4]),
    .nSum4(square_adder_1_nsum0[4]), .SX4(square_barrel_shifter_1_s4), .FX5(SQB_F[5]),
    .nSum5(square_adder_1_nsum0[5]), .SX5(square_barrel_shifter_1_s5), .FX6(SQB_F[6]),
    .nSum6(square_adder_1_nsum0[6]), .SX6(square_barrel_shifter_1_s6), .FX7(SQB_F[7]),
    .nSum7(square_adder_1_nsum0[7]), .SX7(square_barrel_shifter_1_s7), .FX8(SQB_F[8]),
    .nSum8(square_adder_1_nsum0[8]), .SX8(square_barrel_shifter_1_s8), .FX9(SQB_F[9]),
    .nSum9(square_adder_1_nsum0[9]), .SX9(square_barrel_shifter_1_s9), .nCOUT(square_adder_1_ncout),
    .FX10(SQB_F[10]), .SX10(square_barrel_shifter_1_s10), .nSum10(square_adder_1_nsum0[10]));
  nor nor_1 (nor_1_out, nor_3_out, not_3_out, square_sweep_control_1_sw_ovf, NOSQB);
  D_latch d_latch_1 (.EN(nACLK), .D(nor_1_out), .Q(d_latch_1_q));  // open: NOT_Q
  nor nor_2 (nor_2_out, d_latch_1_q, LOCK);
  nor nor_3 (nor_3_out, SQB_F[2], SQB_F[3], SQB_F[4], SQB_F[5], SQB_F[6], SQB_F[7], SQB_F[8], SQB_F[9], SQB_F[10]);
  SQUARE_FREQUENCY_DOWN_COUNTER square_frequency_down_counter_1 (
    .nACLK(nACLK), .ACLK(ACLK), .RES(RES), .PL0(SQB_F[0]), .PL1(SQB_F[1]), .PL2(SQB_F[2]), .PL3(SQB_F[3]),
    .PL4(SQB_F[4]), .PL5(SQB_F[5]), .PL6(SQB_F[6]), .PL7(SQB_F[7]), .PL8(SQB_F[8]), .PL9(SQB_F[9]),
    .PL10(SQB_F[10]), .FQOUT(square_frequency_down_counter_1_fqout),
    .FLOAD(square_frequency_down_counter_1_fload));
  SQUARE_DUTY_DOWN_COUNTER square_duty_down_counter_1 (
    .nACLK(nACLK), .FQOUT(square_frequency_down_counter_1_fqout), .RES(RES), .W4003(W4007),
    .FLOAD(square_frequency_down_counter_1_fload), .W4000(W4004), .D6(D6), .D7(D7),
    .SQOUT(square_duty_down_counter_1_sqout), .SQ_DUTY(SQB_DUTY));
  ENVELOPE_GENERATOR envelope_generator_1 (
    .nACLK(nACLK), .W400_0__4__C(W4004), .W400_3__7__F(W4007), .D0(D0), .D1(D1), .D2(D2), .D3(D3), .D4(D4),
    .D5(D5), .nLFO1(nLFO1), .RES(RES), .V0(SQB0), .V1(SQB1), .V2(SQB2), .V3(SQB3), .nCH_LC(nSQB_LC),
    .CH_IN(nor_2_out), .ENV(SQB_ENV));

  // Notes on the sheet:
  //   Connect to VCC for square0, connect to inverter for square1
  //   !!!
  //   INV5
  //   SW_UVF
endmodule

// SQUARE REGISTER
module SQUARE_REGISTER (
  input  nACLK3,
  input  nACLK,
  input  W4002,
  input  D0,
  input  nSum0,
  input  D1,
  input  nSum1,
  input  D2,
  input  nSum2,
  input  D3,
  input  nSum3,
  input  D4,
  input  nSum4,
  input  D5,
  input  nSum5,
  input  D6,
  input  nSum6,
  input  D7,
  input  nSum7,
  input  nSum8,
  input  nSum9,
  input  nSum10,
  input  DO_SWEEP,
  input  W4003,
  input  D_I,
  output F0,
  output MU0,
  output F1,
  output MU1,
  output F2,
  output MU2,
  output F3,
  output MU3,
  output F4,
  output MU4,
  output F5,
  output MU5,
  output F6,
  output MU6,
  output F7,
  output MU7,
  output F8,
  output MU8,
  output F9,
  output MU9,
  output F10,
  output MU10
);

  wire d_ff_1_q, d_ff_2_q, d_ff_3_q, d_ff_4_q, d_ff_5_q, d_ff_6_q, d_ff_7_q, d_ff_8_q, d_ff_9_q, d_ff_10_q,
       d_ff_11_q, demultiplexer_1_out0, demultiplexer_1_out1, demultiplexer_2_out0, demultiplexer_2_out1,
       demultiplexer_3_out0, demultiplexer_3_out1, demultiplexer_4_out0, demultiplexer_4_out1,
       demultiplexer_5_out0, demultiplexer_5_out1, demultiplexer_6_out0, demultiplexer_6_out1,
       demultiplexer_7_out0, demultiplexer_7_out1, demultiplexer_8_out0, demultiplexer_8_out1,
       demultiplexer_9_out0, demultiplexer_9_out1, demultiplexer_10_out0, demultiplexer_10_out1,
       demultiplexer_11_out0, demultiplexer_11_out1, not_1_out;

  not not_1 (not_1_out, nACLK3);
  D_Flip_Flop #(.trigger("high")) d_ff_1 (.clk(nACLK), .D(nSum0), .Q(d_ff_1_q));  // open: Qn, preset, en, reset
  Demultiplexer #(.enable("false")) demultiplexer_1 (
    .out0(demultiplexer_1_out0), .out1(demultiplexer_1_out1), .in(DO_SWEEP), .sel(d_ff_1_q));
  D_Flip_Flop #(.trigger("high")) d_ff_2 (.clk(nACLK), .D(nSum1), .Q(d_ff_2_q));  // open: Qn, preset, en, reset
  Demultiplexer #(.enable("false")) demultiplexer_2 (
    .out0(demultiplexer_2_out0), .out1(demultiplexer_2_out1), .in(DO_SWEEP), .sel(d_ff_2_q));
  D_Flip_Flop #(.trigger("high")) d_ff_3 (.clk(nACLK), .D(nSum2), .Q(d_ff_3_q));  // open: Qn, preset, en, reset
  Demultiplexer #(.enable("false")) demultiplexer_3 (
    .out0(demultiplexer_3_out0), .out1(demultiplexer_3_out1), .in(DO_SWEEP), .sel(d_ff_3_q));
  D_Flip_Flop #(.trigger("high")) d_ff_4 (.clk(nACLK), .D(nSum3), .Q(d_ff_4_q));  // open: Qn, preset, en, reset
  Demultiplexer #(.enable("false")) demultiplexer_4 (
    .out0(demultiplexer_4_out0), .out1(demultiplexer_4_out1), .in(DO_SWEEP), .sel(d_ff_4_q));
  D_Flip_Flop #(.trigger("high")) d_ff_5 (.clk(nACLK), .D(nSum4), .Q(d_ff_5_q));  // open: Qn, preset, en, reset
  Demultiplexer #(.enable("false")) demultiplexer_5 (
    .out0(demultiplexer_5_out0), .out1(demultiplexer_5_out1), .in(DO_SWEEP), .sel(d_ff_5_q));
  D_Flip_Flop #(.trigger("high")) d_ff_6 (.clk(nACLK), .D(nSum5), .Q(d_ff_6_q));  // open: Qn, preset, en, reset
  Demultiplexer #(.enable("false")) demultiplexer_6 (
    .out0(demultiplexer_6_out0), .out1(demultiplexer_6_out1), .in(DO_SWEEP), .sel(d_ff_6_q));
  D_Flip_Flop #(.trigger("high")) d_ff_7 (.clk(nACLK), .D(nSum6), .Q(d_ff_7_q));  // open: Qn, preset, en, reset
  Demultiplexer #(.enable("false")) demultiplexer_7 (
    .out0(demultiplexer_7_out0), .out1(demultiplexer_7_out1), .in(DO_SWEEP), .sel(d_ff_7_q));
  D_Flip_Flop #(.trigger("high")) d_ff_8 (.clk(nACLK), .D(nSum7), .Q(d_ff_8_q));  // open: Qn, preset, en, reset
  Demultiplexer #(.enable("false")) demultiplexer_8 (
    .out0(demultiplexer_8_out0), .out1(demultiplexer_8_out1), .in(DO_SWEEP), .sel(d_ff_8_q));
  D_Flip_Flop #(.trigger("high")) d_ff_9 (.clk(nACLK), .D(nSum8), .Q(d_ff_9_q));  // open: Qn, preset, en, reset
  Demultiplexer #(.enable("false")) demultiplexer_9 (
    .out0(demultiplexer_9_out0), .out1(demultiplexer_9_out1), .in(DO_SWEEP), .sel(d_ff_9_q));
  D_Flip_Flop #(.trigger("high")) d_ff_10 (.clk(nACLK), .D(nSum9), .Q(d_ff_10_q));  // open: Qn, preset, en, reset
  Demultiplexer #(.enable("false")) demultiplexer_10 (
    .out0(demultiplexer_10_out0), .out1(demultiplexer_10_out1), .in(DO_SWEEP), .sel(d_ff_10_q));
  D_Flip_Flop #(.trigger("high")) d_ff_11 (.clk(nACLK), .D(nSum10), .Q(d_ff_11_q));  // open: Qn, preset, en, reset
  Demultiplexer #(.enable("false")) demultiplexer_11 (
    .out0(demultiplexer_11_out0), .out1(demultiplexer_11_out1), .in(DO_SWEEP), .sel(d_ff_11_q));
  D_Flip_Flop #(.trigger("high")) d_ff_12 (
    .clk(not_1_out), .D(D0), .Q(F0), .preset(demultiplexer_1_out0), .en(W4002), .reset(demultiplexer_1_out1));  // open: Qn
  D_Flip_Flop #(.trigger("high")) d_ff_13 (
    .clk(not_1_out), .D(D1), .Q(F1), .preset(demultiplexer_2_out0), .en(W4002), .reset(demultiplexer_2_out1));  // open: Qn
  D_Flip_Flop #(.trigger("high")) d_ff_14 (
    .clk(not_1_out), .D(D2), .Q(F2), .preset(demultiplexer_3_out0), .en(W4002), .reset(demultiplexer_3_out1));  // open: Qn
  D_Flip_Flop #(.trigger("high")) d_ff_15 (
    .clk(not_1_out), .D(D3), .Q(F3), .preset(demultiplexer_4_out0), .en(W4002), .reset(demultiplexer_4_out1));  // open: Qn
  D_Flip_Flop #(.trigger("high")) d_ff_16 (
    .clk(not_1_out), .D(D4), .Q(F4), .preset(demultiplexer_5_out0), .en(W4002), .reset(demultiplexer_5_out1));  // open: Qn
  D_Flip_Flop #(.trigger("high")) d_ff_17 (
    .clk(not_1_out), .D(D5), .Q(F5), .preset(demultiplexer_6_out0), .en(W4002), .reset(demultiplexer_6_out1));  // open: Qn
  D_Flip_Flop #(.trigger("high")) d_ff_18 (
    .clk(not_1_out), .D(D6), .Q(F6), .preset(demultiplexer_7_out0), .en(W4002), .reset(demultiplexer_7_out1));  // open: Qn
  D_Flip_Flop #(.trigger("high")) d_ff_19 (
    .clk(not_1_out), .D(D7), .Q(F7), .preset(demultiplexer_8_out0), .en(W4002), .reset(demultiplexer_8_out1));  // open: Qn
  D_Flip_Flop #(.trigger("high")) d_ff_20 (
    .clk(not_1_out), .D(D0), .Q(F8), .preset(demultiplexer_9_out0), .en(W4003), .reset(demultiplexer_9_out1));  // open: Qn
  D_Flip_Flop #(.trigger("high")) d_ff_21 (
    .clk(not_1_out), .D(D1), .Q(F9), .preset(demultiplexer_10_out0), .en(W4003), .reset(demultiplexer_10_out1));  // open: Qn
  D_Flip_Flop #(.trigger("high")) d_ff_22 (
    .clk(not_1_out), .D(D2), .Q(F10), .preset(demultiplexer_11_out0), .en(W4003),
    .reset(demultiplexer_11_out1));  // open: Qn
  xor xor_1 (MU0, F0, D_I);
  xor xor_2 (MU1, F1, D_I);
  xor xor_3 (MU2, F2, D_I);
  xor xor_4 (MU3, F3, D_I);
  xor xor_5 (MU4, F4, D_I);
  xor xor_6 (MU5, F5, D_I);
  xor xor_7 (MU6, F6, D_I);
  xor xor_8 (MU7, F7, D_I);
  xor xor_9 (MU8, F8, D_I);
  xor xor_10 (MU9, F9, D_I);
  xor xor_11 (MU10, F10, D_I);

  // Notes on the sheet:
  //   !
  //   W4002 SQUARE0
  //   W4006 SQUARE1
  //   W4003 SQUARE0
  //   W4007 SQUARE1
  //   if /sum 1 reset latch
  //   if /sum 0 preset latch
endmodule

// BARREL SHIFTER
module SQUARE_BARREL_SHIFTER (
  input  MUI0,
  input  MUI1,
  input  MUI2,
  input  MUI3,
  input  MUI4,
  input  MUI5,
  input  MUI6,
  input  MUI7,
  input  MUI8,
  input  MUI9,
  input  MUI10,
  input  Dec_Inc,
  input  SR0,
  input  SR1,
  input  SR2,
  output S0,
  output S1,
  output S2,
  output S3,
  output S4,
  output S5,
  output S6,
  output S7,
  output S8,
  output S9,
  output S10
);

  wire multiplexer_1_out, multiplexer_2_out, multiplexer_3_out, multiplexer_4_out, multiplexer_5_out,
       multiplexer_6_out, multiplexer_7_out, multiplexer_8_out, multiplexer_9_out, multiplexer_10_out,
       multiplexer_11_out, multiplexer_12_out, multiplexer_13_out, multiplexer_14_out, multiplexer_15_out,
       multiplexer_16_out, multiplexer_17_out, multiplexer_18_out, multiplexer_19_out, multiplexer_20_out,
       multiplexer_21_out, multiplexer_22_out;

  Multiplexer #(.enable("false")) multiplexer_1 (.in0(MUI0), .in1(MUI1), .out(multiplexer_1_out), .sel(SR0));
  Multiplexer #(.enable("false")) multiplexer_2 (.in0(MUI1), .in1(MUI2), .out(multiplexer_2_out), .sel(SR0));
  Multiplexer #(.enable("false")) multiplexer_3 (.in0(MUI2), .in1(MUI3), .out(multiplexer_3_out), .sel(SR0));
  Multiplexer #(.enable("false")) multiplexer_4 (.in0(MUI3), .in1(MUI4), .out(multiplexer_4_out), .sel(SR0));
  Multiplexer #(.enable("false")) multiplexer_5 (.in0(MUI4), .in1(MUI5), .out(multiplexer_5_out), .sel(SR0));
  Multiplexer #(.enable("false")) multiplexer_6 (.in0(MUI5), .in1(MUI6), .out(multiplexer_6_out), .sel(SR0));
  Multiplexer #(.enable("false")) multiplexer_7 (.in0(MUI6), .in1(MUI7), .out(multiplexer_7_out), .sel(SR0));
  Multiplexer #(.enable("false")) multiplexer_8 (.in0(MUI7), .in1(MUI8), .out(multiplexer_8_out), .sel(SR0));
  Multiplexer #(.enable("false")) multiplexer_9 (.in0(MUI8), .in1(MUI9), .out(multiplexer_9_out), .sel(SR0));
  Multiplexer #(.enable("false")) multiplexer_10 (.in0(MUI9), .in1(MUI10), .out(multiplexer_10_out), .sel(SR0));
  Multiplexer #(.enable("false")) multiplexer_11 (.in0(MUI10), .in1(Dec_Inc), .out(multiplexer_11_out), .sel(SR0));
  Multiplexer #(.enable("false")) multiplexer_12 (
    .in0(multiplexer_1_out), .in1(multiplexer_3_out), .out(multiplexer_12_out), .sel(SR1));
  Multiplexer #(.enable("false")) multiplexer_13 (
    .in0(multiplexer_2_out), .in1(multiplexer_4_out), .out(multiplexer_13_out), .sel(SR1));
  Multiplexer #(.enable("false")) multiplexer_14 (
    .in0(multiplexer_3_out), .in1(multiplexer_5_out), .out(multiplexer_14_out), .sel(SR1));
  Multiplexer #(.enable("false")) multiplexer_15 (
    .in0(multiplexer_4_out), .in1(multiplexer_6_out), .out(multiplexer_15_out), .sel(SR1));
  Multiplexer #(.enable("false")) multiplexer_16 (
    .in0(multiplexer_5_out), .in1(multiplexer_7_out), .out(multiplexer_16_out), .sel(SR1));
  Multiplexer #(.enable("false")) multiplexer_17 (
    .in0(multiplexer_6_out), .in1(multiplexer_8_out), .out(multiplexer_17_out), .sel(SR1));
  Multiplexer #(.enable("false")) multiplexer_18 (
    .in0(multiplexer_7_out), .in1(multiplexer_9_out), .out(multiplexer_18_out), .sel(SR1));
  Multiplexer #(.enable("false")) multiplexer_19 (
    .in0(multiplexer_8_out), .in1(multiplexer_10_out), .out(multiplexer_19_out), .sel(SR1));
  Multiplexer #(.enable("false")) multiplexer_20 (
    .in0(multiplexer_9_out), .in1(multiplexer_11_out), .out(multiplexer_20_out), .sel(SR1));
  Multiplexer #(.enable("false")) multiplexer_21 (
    .in0(multiplexer_10_out), .in1(Dec_Inc), .out(multiplexer_21_out), .sel(SR1));
  Multiplexer #(.enable("false")) multiplexer_22 (
    .in0(multiplexer_11_out), .in1(Dec_Inc), .out(multiplexer_22_out), .sel(SR1));
  Multiplexer #(.enable("false")) multiplexer_23 (
    .in0(multiplexer_12_out), .in1(multiplexer_16_out), .out(S0), .sel(SR2));
  Multiplexer #(.enable("false")) multiplexer_24 (
    .in0(multiplexer_13_out), .in1(multiplexer_17_out), .out(S1), .sel(SR2));
  Multiplexer #(.enable("false")) multiplexer_25 (
    .in0(multiplexer_14_out), .in1(multiplexer_18_out), .out(S2), .sel(SR2));
  Multiplexer #(.enable("false")) multiplexer_26 (
    .in0(multiplexer_15_out), .in1(multiplexer_19_out), .out(S3), .sel(SR2));
  Multiplexer #(.enable("false")) multiplexer_27 (
    .in0(multiplexer_16_out), .in1(multiplexer_20_out), .out(S4), .sel(SR2));
  Multiplexer #(.enable("false")) multiplexer_28 (
    .in0(multiplexer_17_out), .in1(multiplexer_21_out), .out(S5), .sel(SR2));
  Multiplexer #(.enable("false")) multiplexer_29 (
    .in0(multiplexer_18_out), .in1(multiplexer_22_out), .out(S6), .sel(SR2));
  Multiplexer #(.enable("false")) multiplexer_30 (.in0(multiplexer_19_out), .in1(Dec_Inc), .out(S7), .sel(SR2));
  Multiplexer #(.enable("false")) multiplexer_31 (.in0(multiplexer_20_out), .in1(Dec_Inc), .out(S8), .sel(SR2));
  Multiplexer #(.enable("false")) multiplexer_32 (.in0(multiplexer_21_out), .in1(Dec_Inc), .out(S9), .sel(SR2));
  Multiplexer #(.enable("false")) multiplexer_33 (.in0(multiplexer_22_out), .in1(Dec_Inc), .out(S10), .sel(SR2));
endmodule

// SQUARE ADDER
module SQUARE_ADDER (
  input  nCIN,
  input  FX0,
  input  SX0,
  input  FX1,
  input  SX1,
  input  FX2,
  input  SX2,
  input  FX3,
  input  SX3,
  input  FX4,
  input  SX4,
  input  FX5,
  input  SX5,
  input  FX6,
  input  SX6,
  input  FX7,
  input  SX7,
  input  FX8,
  input  SX8,
  input  FX9,
  input  SX9,
  input  FX10,
  input  SX10,
  output nSum0,
  output nSum1,
  output nSum2,
  output nSum3,
  output nSum4,
  output nSum5,
  output nSum6,
  output nSum7,
  output nSum8,
  output nSum9,
  output nSum10,
  output nCOUT
);

  wire and_1_out, and_2_out, and_3_out, and_4_out, and_5_out, and_6_out, and_7_out, and_8_out, and_9_out,
       and_10_out, and_11_out, and_12_out, and_13_out, and_14_out, and_15_out, and_16_out, and_17_out,
       and_18_out, and_19_out, and_20_out, and_21_out, and_22_out, and_23_out, and_24_out, and_25_out,
       and_26_out, and_27_out, and_28_out, and_29_out, and_30_out, and_31_out, and_32_out, and_33_out,
       and_34_out, and_35_out, and_36_out, and_37_out, and_38_out, and_39_out, and_40_out, and_41_out,
       and_42_out, and_43_out, and_44_out, and_45_out, and_46_out, and_47_out, and_48_out, and_49_out,
       and_50_out, and_51_out, and_52_out, and_53_out, and_54_out, and_55_out, and_56_out, and_57_out,
       and_58_out, and_59_out, and_60_out, and_61_out, and_62_out, and_63_out, and_64_out, and_65_out,
       and_66_out, and_67_out, and_68_out, and_69_out, and_70_out, and_71_out, and_72_out, and_73_out,
       and_74_out, and_75_out, and_76_out, and_77_out, nor_1_out, nor_2_out, nor_3_out, nor_4_out, nor_5_out,
       nor_6_out, nor_7_out, nor_8_out, nor_9_out, nor_10_out, not_1_out, not_2_out, not_3_out, not_4_out,
       not_5_out, not_6_out, not_7_out, not_8_out, not_9_out, not_10_out, not_11_out, not_12_out, not_13_out,
       not_14_out, not_15_out, not_16_out, not_17_out, not_18_out, not_19_out, not_20_out, not_21_out,
       not_22_out, not_23_out, not_24_out, not_25_out, not_26_out, not_27_out, not_28_out, not_29_out,
       not_30_out, not_31_out, not_32_out, not_33_out;

  not not_1 (not_1_out, FX0);
  not not_2 (not_2_out, FX1);
  not not_3 (not_3_out, FX2);
  not not_4 (not_4_out, FX3);
  not not_5 (not_5_out, FX4);
  not not_6 (not_6_out, FX5);
  not not_7 (not_7_out, FX6);
  not not_8 (not_8_out, FX7);
  not not_9 (not_9_out, FX8);
  not not_10 (not_10_out, FX9);
  not not_11 (not_11_out, FX10);
  not not_12 (not_12_out, nCIN);
  not not_13 (not_13_out, SX0);
  and and_1 (and_1_out, SX0, FX0);
  not not_14 (not_14_out, nor_1_out);
  not not_15 (not_15_out, SX1);
  and and_2 (and_2_out, SX1, FX1);
  not not_16 (not_16_out, nor_2_out);
  not not_17 (not_17_out, SX2);
  and and_3 (and_3_out, SX2, FX2);
  not not_18 (not_18_out, nor_3_out);
  not not_19 (not_19_out, SX3);
  and and_4 (and_4_out, SX3, FX3);
  not not_20 (not_20_out, nor_4_out);
  not not_21 (not_21_out, SX4);
  and and_5 (and_5_out, SX4, FX4);
  not not_22 (not_22_out, nor_5_out);
  not not_23 (not_23_out, SX5);
  and and_6 (and_6_out, SX5, FX5);
  not not_24 (not_24_out, nor_6_out);
  not not_25 (not_25_out, SX6);
  and and_7 (and_7_out, SX6, FX6);
  not not_26 (not_26_out, nor_7_out);
  not not_27 (not_27_out, SX7);
  and and_8 (and_8_out, SX7, FX7);
  not not_28 (not_28_out, nor_8_out);
  not not_29 (not_29_out, SX8);
  and and_9 (and_9_out, SX8, FX8);
  not not_30 (not_30_out, nor_9_out);
  not not_31 (not_31_out, SX9);
  and and_10 (and_10_out, SX9, FX9);
  not not_32 (not_32_out, nor_10_out);
  not not_33 (not_33_out, SX10);
  and and_11 (and_11_out, SX10, FX10);
  and and_12 (and_12_out, SX0, not_1_out, not_12_out);
  and and_13 (and_13_out, not_13_out, not_12_out, FX0);
  nor nor_1 (nor_1_out, and_1_out, and_13_out, and_12_out);
  and and_14 (and_14_out, SX1, not_2_out, not_14_out);
  and and_15 (and_15_out, not_15_out, not_14_out, FX1);
  nor nor_2 (nor_2_out, and_2_out, and_15_out, and_14_out);
  and and_16 (and_16_out, SX2, not_3_out, not_16_out);
  and and_17 (and_17_out, not_17_out, not_16_out, FX2);
  nor nor_3 (nor_3_out, and_3_out, and_17_out, and_16_out);
  and and_18 (and_18_out, SX3, not_4_out, not_18_out);
  and and_19 (and_19_out, not_19_out, not_18_out, FX3);
  nor nor_4 (nor_4_out, and_4_out, and_19_out, and_18_out);
  and and_20 (and_20_out, SX4, not_5_out, not_20_out);
  and and_21 (and_21_out, not_21_out, not_20_out, FX4);
  nor nor_5 (nor_5_out, and_5_out, and_21_out, and_20_out);
  and and_22 (and_22_out, not_23_out, not_22_out, FX5);
  and and_23 (and_23_out, SX5, not_6_out, not_22_out);
  nor nor_6 (nor_6_out, and_6_out, and_22_out, and_23_out);
  and and_24 (and_24_out, SX6, not_7_out, not_24_out);
  and and_25 (and_25_out, not_25_out, not_24_out, FX6);
  nor nor_7 (nor_7_out, and_7_out, and_25_out, and_24_out);
  and and_26 (and_26_out, not_27_out, not_26_out, FX7);
  and and_27 (and_27_out, SX7, not_8_out, not_26_out);
  nor nor_8 (nor_8_out, and_8_out, and_26_out, and_27_out);
  and and_28 (and_28_out, not_29_out, not_28_out, FX8);
  and and_29 (and_29_out, SX8, not_9_out, not_28_out);
  nor nor_9 (nor_9_out, and_9_out, and_28_out, and_29_out);
  and and_30 (and_30_out, SX9, not_10_out, not_30_out);
  and and_31 (and_31_out, not_31_out, not_30_out, FX9);
  nor nor_10 (nor_10_out, and_10_out, and_31_out, and_30_out);
  and and_32 (and_32_out, not_33_out, not_32_out, FX10);
  and and_33 (and_33_out, SX10, not_11_out, not_32_out);
  nor nor_11 (nCOUT, and_11_out, and_32_out, and_33_out);
  and and_34 (and_34_out, not_13_out, FX0, nCIN);
  and and_35 (and_35_out, not_15_out, FX1, nor_1_out);
  and and_36 (and_36_out, not_17_out, FX2, nor_2_out);
  and and_37 (and_37_out, not_19_out, FX3, nor_3_out);
  and and_38 (and_38_out, not_21_out, FX4, nor_4_out);
  and and_39 (and_39_out, not_23_out, FX5, nor_5_out);
  and and_40 (and_40_out, not_25_out, FX6, nor_6_out);
  and and_41 (and_41_out, not_27_out, FX7, nor_7_out);
  and and_42 (and_42_out, not_29_out, FX8, nor_8_out);
  and and_43 (and_43_out, not_31_out, FX9, nor_9_out);
  and and_44 (and_44_out, not_33_out, FX10, nor_10_out);
  and and_45 (and_45_out, not_13_out, not_1_out, not_12_out);
  and and_46 (and_46_out, SX0, not_1_out, nCIN);
  nor nor_12 (nSum0, and_34_out, and_46_out, and_45_out, and_67_out);
  and and_47 (and_47_out, SX1, not_2_out, nor_1_out);
  and and_48 (and_48_out, not_15_out, not_2_out, not_14_out);
  nor nor_13 (nSum1, and_35_out, and_47_out, and_48_out, and_68_out);
  and and_49 (and_49_out, SX2, not_3_out, nor_2_out);
  and and_50 (and_50_out, not_17_out, not_3_out, not_16_out);
  nor nor_14 (nSum2, and_36_out, and_49_out, and_50_out, and_69_out);
  and and_51 (and_51_out, SX3, not_4_out, nor_3_out);
  and and_52 (and_52_out, not_19_out, not_4_out, not_18_out);
  nor nor_15 (nSum3, and_37_out, and_51_out, and_52_out, and_70_out);
  and and_53 (and_53_out, not_21_out, not_5_out, not_20_out);
  and and_54 (and_54_out, SX4, not_5_out, nor_4_out);
  nor nor_16 (nSum4, and_38_out, and_54_out, and_53_out, and_71_out);
  and and_55 (and_55_out, SX5, not_6_out, nor_5_out);
  and and_56 (and_56_out, not_23_out, not_6_out, not_22_out);
  nor nor_17 (nSum5, and_39_out, and_55_out, and_56_out, and_72_out);
  and and_57 (and_57_out, SX6, not_7_out, nor_6_out);
  and and_58 (and_58_out, not_25_out, not_7_out, not_24_out);
  nor nor_18 (nSum6, and_40_out, and_57_out, and_58_out, and_73_out);
  and and_59 (and_59_out, not_27_out, not_8_out, not_26_out);
  and and_60 (and_60_out, SX7, not_8_out, nor_7_out);
  nor nor_19 (nSum7, and_41_out, and_60_out, and_59_out, and_74_out);
  and and_61 (and_61_out, not_29_out, not_9_out, not_28_out);
  and and_62 (and_62_out, SX8, not_9_out, nor_8_out);
  nor nor_20 (nSum8, and_42_out, and_62_out, and_61_out, and_75_out);
  and and_63 (and_63_out, not_31_out, not_10_out, not_30_out);
  and and_64 (and_64_out, SX9, not_10_out, nor_9_out);
  nor nor_21 (nSum9, and_43_out, and_64_out, and_63_out, and_76_out);
  and and_65 (and_65_out, SX10, not_11_out, nor_10_out);
  and and_66 (and_66_out, not_33_out, not_11_out, not_32_out);
  nor nor_22 (nSum10, and_44_out, and_65_out, and_66_out, and_77_out);
  and and_67 (and_67_out, SX0, not_12_out, FX0);
  and and_68 (and_68_out, SX1, not_14_out, FX1);
  and and_69 (and_69_out, SX2, not_16_out, FX2);
  and and_70 (and_70_out, SX3, not_18_out, FX3);
  and and_71 (and_71_out, SX4, not_20_out, FX4);
  and and_72 (and_72_out, SX5, not_22_out, FX5);
  and and_73 (and_73_out, SX6, not_24_out, FX6);
  and and_74 (and_74_out, SX7, not_26_out, FX7);
  and and_75 (and_75_out, SX8, not_28_out, FX8);
  and and_76 (and_76_out, SX9, not_30_out, FX9);
  and and_77 (and_77_out, SX10, not_32_out, FX10);
endmodule

// SWEEP CONTROL
module SQUARE_SWEEP_CONTROL (
  input  nACLK,
  input  nCOUT,
  input  D0,
  input  D1,
  input  D2,
  input  D3,
  input  D7,
  input  SW_UVF,
  input  NOSQA,
  input  nLFO2,
  input  RES,
  input  D4,
  input  D5,
  input  D6,
  input  W400x,
  output [7:0] SWEEP_REG,
  output SW_OVF,
  output SR0,
  output SR1,
  output SR2,
  output D_I,
  output DO_SWEEP
);

  wire d_ff_5_qn, d_ff_9_q, d_ff_9_qn, d_ff_10_q, d_ff_10_qn, d_ff_11_q, d_ff_11_qn, d_ff_12_qn, d_ff_13_qn,
       d_ff_14_qn, d_latch_1_not_q, d_latch_1_q, d_latch_2_not_q, d_latch_2_q, demultiplexer_1_out0,
       demultiplexer_1_out1, demultiplexer_2_out0, demultiplexer_2_out1, demultiplexer_3_out0,
       demultiplexer_3_out1, nor_1_out, nor_2_out, nor_3_out, nor_4_out, nor_5_out, nor_6_out, nor_7_out,
       nor_8_out, nor_10_out, nor_11_out, not_1_out, not_2_out, not_3_out, not_4_out, not_5_out, or_1_out,
       or_2_out, or_3_out, xor_1_out, xor_2_out, xor_3_out;

  not not_1 (not_1_out, nACLK);
  D_Flip_Flop #(.trigger("high")) d_ff_1 (.clk(not_1_out), .D(D0), .Q(SR0), .en(W400x));  // open: Qn, preset, reset
  D_Flip_Flop #(.trigger("high")) d_ff_2 (.clk(not_1_out), .D(D1), .Q(SR1), .en(W400x));  // open: Qn, preset, reset
  D_Flip_Flop #(.trigger("high")) d_ff_3 (.clk(not_1_out), .D(D2), .Q(SR2), .en(W400x));  // open: Qn, preset, reset
  D_Flip_Flop #(.trigger("high")) d_ff_4 (.clk(not_1_out), .D(D3), .Q(D_I), .en(W400x));  // open: Qn, preset, reset
  D_Flip_Flop #(.trigger("high")) d_ff_5 (
    .clk(not_1_out), .D(D7), .Q(SWEEP_REG[7]), .Qn(d_ff_5_qn), .en(W400x));  // open: preset, reset
  D_Flip_Flop #(.trigger("high")) d_ff_6 (
    .clk(not_1_out), .D(D4), .Q(SWEEP_REG[4]), .en(W400x));  // open: Qn, preset, reset
  D_Flip_Flop #(.trigger("high")) d_ff_7 (
    .clk(not_1_out), .D(D5), .Q(SWEEP_REG[5]), .en(W400x));  // open: Qn, preset, reset
  D_Flip_Flop #(.trigger("high")) d_ff_8 (
    .clk(not_1_out), .D(D6), .Q(SWEEP_REG[6]), .en(W400x));  // open: Qn, preset, reset
  Demultiplexer #(.enable("false")) demultiplexer_1 (
    .out0(demultiplexer_1_out0), .out1(demultiplexer_1_out1), .in(nor_8_out), .sel(SWEEP_REG[4]));
  Demultiplexer #(.enable("false")) demultiplexer_2 (
    .out0(demultiplexer_2_out0), .out1(demultiplexer_2_out1), .in(nor_8_out), .sel(SWEEP_REG[5]));
  Demultiplexer #(.enable("false")) demultiplexer_3 (
    .out0(demultiplexer_3_out0), .out1(demultiplexer_3_out1), .in(nor_8_out), .sel(SWEEP_REG[6]));
  or or_1 (or_1_out, RES, demultiplexer_1_out0);
  or or_2 (or_2_out, RES, demultiplexer_2_out0);
  or or_3 (or_3_out, RES, demultiplexer_3_out0);
  nor nor_1 (nor_1_out, d_latch_1_q, nLFO2);
  D_Flip_Flop #(.trigger("high")) d_ff_9 (
    .clk(nor_7_out), .D(d_ff_12_qn), .Q(d_ff_9_q), .Qn(d_ff_9_qn), .preset(demultiplexer_1_out1),
    .reset(or_1_out));  // open: en
  D_Flip_Flop #(.trigger("high")) d_ff_10 (
    .clk(nor_7_out), .D(d_ff_13_qn), .Q(d_ff_10_q), .Qn(d_ff_10_qn), .preset(demultiplexer_2_out1),
    .reset(or_2_out));  // open: en
  D_Flip_Flop #(.trigger("high")) d_ff_11 (
    .clk(nor_7_out), .D(d_ff_14_qn), .Q(d_ff_11_q), .Qn(d_ff_11_qn), .preset(demultiplexer_3_out1),
    .reset(or_3_out));  // open: en
  nor nor_2 (nor_2_out, nor_1_out, nor_3_out);
  nor nor_3 (nor_3_out, nor_2_out, W400x);
  xor xor_1 (xor_1_out, 1'b1, d_ff_9_qn);
  not not_2 (not_2_out, 1'b1);
  nor nor_4 (nor_4_out, not_2_out, d_ff_9_q);
  xor xor_2 (xor_2_out, nor_4_out, d_ff_10_qn);
  not not_3 (not_3_out, nor_4_out);
  nor nor_5 (nor_5_out, not_3_out, d_ff_10_q);
  xor xor_3 (xor_3_out, nor_5_out, d_ff_11_qn);
  not not_4 (not_4_out, nor_5_out);
  nor nor_6 (nor_6_out, not_4_out, d_ff_11_q);
  nor nor_7 (nor_7_out, not_5_out, nLFO2);
  nor nor_8 (nor_8_out, nLFO2, nor_11_out);
  nor nor_9 (SW_OVF, nCOUT, D_I);
  not not_5 (not_5_out, nor_11_out);
  D_Flip_Flop #(.trigger("high")) d_ff_12 (.clk(nACLK), .D(xor_1_out), .Qn(d_ff_12_qn));  // open: Q, preset, en, reset
  D_Flip_Flop #(.trigger("high")) d_ff_13 (.clk(nACLK), .D(xor_2_out), .Qn(d_ff_13_qn));  // open: Q, preset, en, reset
  D_Flip_Flop #(.trigger("high")) d_ff_14 (.clk(nACLK), .D(xor_3_out), .Qn(d_ff_14_qn));  // open: Q, preset, en, reset
  D_latch d_latch_1 (.EN(nACLK), .D(nor_3_out), .Q(d_latch_1_q), .NOT_Q(d_latch_1_not_q));
  nor nor_10 (nor_10_out, SR2, SR1, SR0);
  D_latch d_latch_2 (.EN(nACLK), .D(nor_6_out), .Q(d_latch_2_q), .NOT_Q(d_latch_2_not_q));
  nor nor_11 (nor_11_out, d_latch_2_q, d_latch_1_not_q);
  nor nor_12 (DO_SWEEP, nor_10_out, SW_OVF, d_ff_5_qn, SW_UVF, NOSQA, nLFO2, d_latch_2_not_q);

  assign SWEEP_REG[3:0] = {D_I, SR2, SR1, SR0};

  // Notes on the sheet:
  //   W4001 SQUARE0
  //   W4005 SQUARE1
  //   SR0
  //   SR1
  //   SR2
  //   DEC/INC
  //   SWDIS
  //   P0
  //   P1
  //   P2
  //   R
  //   NOR2
  //   S
  //   SWEEP DOWN COUNTER
  //   SSTEP
  //   SLOAD
  //   Q
  //   NORFF1
  //   RS1
  //   NORFF2
  //   /Q
  //   NOR1
  //   DL1
  //   SRZ
  //   /SCO
  //   DL3
  //   NOR7
  //   SWEEPRELOAD
  //   NOR3
  //   NOR4
endmodule

// SQUARE FREQUENCY COUNTER
module SQUARE_FREQUENCY_DOWN_COUNTER (
  input  nACLK,
  input  RES,
  input  PL0,
  input  PL1,
  input  PL2,
  input  PL3,
  input  PL4,
  input  PL5,
  input  PL6,
  input  PL7,
  input  PL8,
  input  PL9,
  input  PL10,
  input  ACLK,
  output FQOUT,
  output FLOAD
);

  wire d_ff_1_q, d_ff_1_qn, d_ff_2_q, d_ff_2_qn, d_ff_3_q, d_ff_3_qn, d_ff_4_q, d_ff_4_qn, d_ff_5_q,
       d_ff_5_qn, d_ff_6_q, d_ff_6_qn, d_ff_7_q, d_ff_7_qn, d_ff_8_q, d_ff_8_qn, d_ff_9_q, d_ff_9_qn,
       d_ff_10_q, d_ff_10_qn, d_ff_11_q, d_ff_11_qn, d_ff_12_qn, d_ff_13_qn, d_ff_14_qn, d_ff_15_qn,
       d_ff_16_qn, d_ff_17_qn, d_ff_18_qn, d_ff_19_qn, d_ff_20_qn, d_ff_21_qn, d_ff_22_qn, d_latch_1_not_q,
       demultiplexer_1_out0, demultiplexer_1_out1, demultiplexer_2_out0, demultiplexer_2_out1,
       demultiplexer_3_out0, demultiplexer_3_out1, demultiplexer_4_out0, demultiplexer_4_out1,
       demultiplexer_5_out0, demultiplexer_5_out1, demultiplexer_6_out0, demultiplexer_6_out1,
       demultiplexer_7_out0, demultiplexer_7_out1, demultiplexer_8_out0, demultiplexer_8_out1,
       demultiplexer_9_out0, demultiplexer_9_out1, demultiplexer_10_out0, demultiplexer_10_out1,
       demultiplexer_11_out0, demultiplexer_11_out1, nor_2_out, nor_3_out, nor_4_out, nor_5_out, nor_6_out,
       nor_7_out, nor_8_out, nor_9_out, nor_10_out, nor_11_out, nor_12_out, not_1_out, not_2_out, not_3_out,
       not_4_out, not_5_out, not_6_out, not_7_out, not_8_out, not_9_out, not_10_out, not_11_out, not_12_out,
       or_1_out, or_2_out, or_3_out, or_4_out, or_5_out, or_6_out, or_7_out, or_8_out, or_9_out, or_10_out,
       or_11_out, xor_1_out, xor_2_out, xor_3_out, xor_4_out, xor_5_out, xor_6_out, xor_7_out, xor_8_out,
       xor_9_out, xor_10_out, xor_11_out;

  Demultiplexer #(.enable("false")) demultiplexer_1 (
    .out0(demultiplexer_1_out0), .out1(demultiplexer_1_out1), .in(FLOAD), .sel(PL0));
  Demultiplexer #(.enable("false")) demultiplexer_2 (
    .out0(demultiplexer_2_out0), .out1(demultiplexer_2_out1), .in(FLOAD), .sel(PL1));
  Demultiplexer #(.enable("false")) demultiplexer_3 (
    .out0(demultiplexer_3_out0), .out1(demultiplexer_3_out1), .in(FLOAD), .sel(PL2));
  Demultiplexer #(.enable("false")) demultiplexer_4 (
    .out0(demultiplexer_4_out0), .out1(demultiplexer_4_out1), .in(FLOAD), .sel(PL3));
  Demultiplexer #(.enable("false")) demultiplexer_5 (
    .out0(demultiplexer_5_out0), .out1(demultiplexer_5_out1), .in(FLOAD), .sel(PL4));
  Demultiplexer #(.enable("false")) demultiplexer_6 (
    .out0(demultiplexer_6_out0), .out1(demultiplexer_6_out1), .in(FLOAD), .sel(PL5));
  Demultiplexer #(.enable("false")) demultiplexer_7 (
    .out0(demultiplexer_7_out0), .out1(demultiplexer_7_out1), .in(FLOAD), .sel(PL6));
  Demultiplexer #(.enable("false")) demultiplexer_8 (
    .out0(demultiplexer_8_out0), .out1(demultiplexer_8_out1), .in(FLOAD), .sel(PL7));
  Demultiplexer #(.enable("false")) demultiplexer_9 (
    .out0(demultiplexer_9_out0), .out1(demultiplexer_9_out1), .in(FLOAD), .sel(PL8));
  Demultiplexer #(.enable("false")) demultiplexer_10 (
    .out0(demultiplexer_10_out0), .out1(demultiplexer_10_out1), .in(FLOAD), .sel(PL9));
  Demultiplexer #(.enable("false")) demultiplexer_11 (
    .out0(demultiplexer_11_out0), .out1(demultiplexer_11_out1), .in(FLOAD), .sel(PL10));
  or or_1 (or_1_out, RES, demultiplexer_1_out0);
  or or_2 (or_2_out, RES, demultiplexer_2_out0);
  or or_3 (or_3_out, RES, demultiplexer_3_out0);
  or or_4 (or_4_out, RES, demultiplexer_4_out0);
  or or_5 (or_5_out, RES, demultiplexer_5_out0);
  or or_6 (or_6_out, RES, demultiplexer_6_out0);
  or or_7 (or_7_out, RES, demultiplexer_7_out0);
  or or_8 (or_8_out, RES, demultiplexer_8_out0);
  or or_9 (or_9_out, RES, demultiplexer_9_out0);
  or or_10 (or_10_out, RES, demultiplexer_10_out0);
  or or_11 (or_11_out, RES, demultiplexer_11_out0);
  D_Flip_Flop #(.trigger("high")) d_ff_1 (
    .clk(nor_2_out), .D(d_ff_12_qn), .Q(d_ff_1_q), .Qn(d_ff_1_qn), .preset(demultiplexer_1_out1),
    .reset(or_1_out));  // open: en
  D_Flip_Flop #(.trigger("high")) d_ff_2 (
    .clk(nor_2_out), .D(d_ff_13_qn), .Q(d_ff_2_q), .Qn(d_ff_2_qn), .preset(demultiplexer_2_out1),
    .reset(or_2_out));  // open: en
  D_Flip_Flop #(.trigger("high")) d_ff_3 (
    .clk(nor_2_out), .D(d_ff_14_qn), .Q(d_ff_3_q), .Qn(d_ff_3_qn), .preset(demultiplexer_3_out1),
    .reset(or_3_out));  // open: en
  D_Flip_Flop #(.trigger("high")) d_ff_4 (
    .clk(nor_2_out), .D(d_ff_15_qn), .Q(d_ff_4_q), .Qn(d_ff_4_qn), .preset(demultiplexer_4_out1),
    .reset(or_4_out));  // open: en
  D_Flip_Flop #(.trigger("high")) d_ff_5 (
    .clk(nor_2_out), .D(d_ff_16_qn), .Q(d_ff_5_q), .Qn(d_ff_5_qn), .preset(demultiplexer_5_out1),
    .reset(or_5_out));  // open: en
  D_Flip_Flop #(.trigger("high")) d_ff_6 (
    .clk(nor_2_out), .D(d_ff_17_qn), .Q(d_ff_6_q), .Qn(d_ff_6_qn), .preset(demultiplexer_6_out1),
    .reset(or_6_out));  // open: en
  D_Flip_Flop #(.trigger("high")) d_ff_7 (
    .clk(nor_2_out), .D(d_ff_18_qn), .Q(d_ff_7_q), .Qn(d_ff_7_qn), .preset(demultiplexer_7_out1),
    .reset(or_7_out));  // open: en
  D_Flip_Flop #(.trigger("high")) d_ff_8 (
    .clk(nor_2_out), .D(d_ff_19_qn), .Q(d_ff_8_q), .Qn(d_ff_8_qn), .preset(demultiplexer_8_out1),
    .reset(or_8_out));  // open: en
  D_Flip_Flop #(.trigger("high")) d_ff_9 (
    .clk(nor_2_out), .D(d_ff_20_qn), .Q(d_ff_9_q), .Qn(d_ff_9_qn), .preset(demultiplexer_9_out1),
    .reset(or_9_out));  // open: en
  D_Flip_Flop #(.trigger("high")) d_ff_10 (
    .clk(nor_2_out), .D(d_ff_21_qn), .Q(d_ff_10_q), .Qn(d_ff_10_qn), .preset(demultiplexer_10_out1),
    .reset(or_10_out));  // open: en
  D_Flip_Flop #(.trigger("high")) d_ff_11 (
    .clk(nor_2_out), .D(d_ff_22_qn), .Q(d_ff_11_q), .Qn(d_ff_11_qn), .preset(demultiplexer_11_out1),
    .reset(or_11_out));  // open: en
  nor nor_1 (FLOAD, d_latch_1_not_q, ACLK);
  nor nor_2 (nor_2_out, ACLK, not_1_out);
  not not_1 (not_1_out, d_latch_1_not_q);
  xor xor_1 (xor_1_out, 1'b1, d_ff_1_qn);
  not not_2 (not_2_out, 1'b1);
  nor nor_3 (nor_3_out, not_2_out, d_ff_1_q);
  xor xor_2 (xor_2_out, nor_3_out, d_ff_2_qn);
  not not_3 (not_3_out, nor_3_out);
  nor nor_4 (nor_4_out, not_3_out, d_ff_2_q);
  xor xor_3 (xor_3_out, nor_4_out, d_ff_3_qn);
  not not_4 (not_4_out, nor_4_out);
  nor nor_5 (nor_5_out, not_4_out, d_ff_3_q);
  xor xor_4 (xor_4_out, nor_5_out, d_ff_4_qn);
  not not_5 (not_5_out, nor_5_out);
  nor nor_6 (nor_6_out, not_5_out, d_ff_4_q);
  xor xor_5 (xor_5_out, nor_6_out, d_ff_5_qn);
  not not_6 (not_6_out, nor_6_out);
  nor nor_7 (nor_7_out, not_6_out, d_ff_5_q);
  xor xor_6 (xor_6_out, nor_7_out, d_ff_6_qn);
  not not_7 (not_7_out, nor_7_out);
  nor nor_8 (nor_8_out, not_7_out, d_ff_6_q);
  xor xor_7 (xor_7_out, nor_8_out, d_ff_7_qn);
  not not_8 (not_8_out, nor_8_out);
  nor nor_9 (nor_9_out, not_8_out, d_ff_7_q);
  xor xor_8 (xor_8_out, nor_9_out, d_ff_8_qn);
  not not_9 (not_9_out, nor_9_out);
  nor nor_10 (nor_10_out, not_9_out, d_ff_8_q);
  xor xor_9 (xor_9_out, nor_10_out, d_ff_9_qn);
  not not_10 (not_10_out, nor_10_out);
  nor nor_11 (nor_11_out, not_10_out, d_ff_9_q);
  xor xor_10 (xor_10_out, nor_11_out, d_ff_10_qn);
  not not_11 (not_11_out, nor_11_out);
  nor nor_12 (nor_12_out, not_11_out, d_ff_10_q);
  xor xor_11 (xor_11_out, nor_12_out, d_ff_11_qn);
  not not_12 (not_12_out, nor_12_out);
  nor nor_13 (FQOUT, not_12_out, d_ff_11_q);
  D_Flip_Flop #(.trigger("high")) d_ff_12 (.clk(nACLK), .D(xor_1_out), .Qn(d_ff_12_qn));  // open: Q, preset, en, reset
  D_Flip_Flop #(.trigger("high")) d_ff_13 (.clk(nACLK), .D(xor_2_out), .Qn(d_ff_13_qn));  // open: Q, preset, en, reset
  D_Flip_Flop #(.trigger("high")) d_ff_14 (.clk(nACLK), .D(xor_3_out), .Qn(d_ff_14_qn));  // open: Q, preset, en, reset
  D_Flip_Flop #(.trigger("high")) d_ff_15 (.clk(nACLK), .D(xor_4_out), .Qn(d_ff_15_qn));  // open: Q, preset, en, reset
  D_Flip_Flop #(.trigger("high")) d_ff_16 (.clk(nACLK), .D(xor_5_out), .Qn(d_ff_16_qn));  // open: Q, preset, en, reset
  D_Flip_Flop #(.trigger("high")) d_ff_17 (.clk(nACLK), .D(xor_6_out), .Qn(d_ff_17_qn));  // open: Q, preset, en, reset
  D_Flip_Flop #(.trigger("high")) d_ff_18 (.clk(nACLK), .D(xor_7_out), .Qn(d_ff_18_qn));  // open: Q, preset, en, reset
  D_Flip_Flop #(.trigger("high")) d_ff_19 (.clk(nACLK), .D(xor_8_out), .Qn(d_ff_19_qn));  // open: Q, preset, en, reset
  D_Flip_Flop #(.trigger("high")) d_ff_20 (.clk(nACLK), .D(xor_9_out), .Qn(d_ff_20_qn));  // open: Q, preset, en, reset
  D_Flip_Flop #(.trigger("high")) d_ff_21 (.clk(nACLK), .D(xor_10_out), .Qn(d_ff_21_qn));  // open: Q, preset, en, reset
  D_Flip_Flop #(.trigger("high")) d_ff_22 (.clk(nACLK), .D(xor_11_out), .Qn(d_ff_22_qn));  // open: Q, preset, en, reset
  D_latch d_latch_1 (.EN(nACLK), .D(FQOUT), .NOT_Q(d_latch_1_not_q));  // open: Q

  // Notes on the sheet:
  //   FLOAD
  //   FSTEP
  //   INV2
  //   DL4
endmodule

// DUTY DOWN COUNTER
module SQUARE_DUTY_DOWN_COUNTER (
  input  nACLK,
  input  FQOUT,
  input  RES,
  input  W4003,
  input  FLOAD,
  input  D6,
  input  D7,
  input  W4000,
  output SQOUT,
  output [1:0] SQ_DUTY
);

  wire d_ff_1_q, d_ff_1_qn, d_ff_2_q, d_ff_2_qn, d_ff_3_q, d_ff_3_qn, d_ff_6_qn, d_ff_7_qn, d_ff_8_qn,
       nand_1_out, nor_1_out, nor_2_out, nor_3_out, nor_4_out, not_1_out, not_2_out, not_3_out, not_4_out,
       not_5_out, not_6_out, or_1_out, xor_1_out, xor_2_out, xor_3_out;

  or or_1 (or_1_out, RES, W4003);
  D_Flip_Flop #(.trigger("high")) d_ff_1 (
    .clk(FLOAD), .D(d_ff_6_qn), .Q(d_ff_1_q), .Qn(d_ff_1_qn), .reset(or_1_out));  // open: preset, en
  D_Flip_Flop #(.trigger("high")) d_ff_2 (
    .clk(FLOAD), .D(d_ff_7_qn), .Q(d_ff_2_q), .Qn(d_ff_2_qn), .reset(or_1_out));  // open: preset, en
  D_Flip_Flop #(.trigger("high")) d_ff_3 (
    .clk(FLOAD), .D(d_ff_8_qn), .Q(d_ff_3_q), .Qn(d_ff_3_qn), .reset(or_1_out));  // open: preset, en
  D_Flip_Flop #(.trigger("high")) d_ff_4 (
    .clk(not_4_out), .D(D6), .Q(SQ_DUTY[0]), .en(W4000));  // open: Qn, preset, reset
  D_Flip_Flop #(.trigger("high")) d_ff_5 (
    .clk(not_4_out), .D(D7), .Q(SQ_DUTY[1]), .en(W4000));  // open: Qn, preset, reset
  not not_1 (not_1_out, FQOUT);
  not not_2 (not_2_out, nor_1_out);
  not not_3 (not_3_out, nor_2_out);
  not not_4 (not_4_out, nACLK);
  xor xor_1 (xor_1_out, FQOUT, d_ff_1_qn);
  nor nor_1 (nor_1_out, not_1_out, d_ff_1_q);
  xor xor_2 (xor_2_out, nor_1_out, d_ff_2_qn);
  nor nor_2 (nor_2_out, not_2_out, d_ff_2_q);
  xor xor_3 (xor_3_out, nor_2_out, d_ff_3_qn);
  nor nor_3 (nor_3_out, not_3_out, d_ff_3_q);
  D_Flip_Flop #(.trigger("high")) d_ff_6 (.clk(nACLK), .D(xor_1_out), .Qn(d_ff_6_qn));  // open: Q, preset, en, reset
  D_Flip_Flop #(.trigger("high")) d_ff_7 (.clk(nACLK), .D(xor_2_out), .Qn(d_ff_7_qn));  // open: Q, preset, en, reset
  D_Flip_Flop #(.trigger("high")) d_ff_8 (.clk(nACLK), .D(xor_3_out), .Qn(d_ff_8_qn));  // open: Q, preset, en, reset
  not not_5 (not_5_out, d_ff_1_q);
  nand nand_1 (nand_1_out, d_ff_2_q, d_ff_3_q);
  nor nor_4 (nor_4_out, not_5_out, nand_1_out);
  not not_6 (not_6_out, nand_1_out);
  Multiplexer #(.select(2), .enable("false")) multiplexer_1 (
    .in0(nor_4_out), .in1(not_6_out), .in2(d_ff_3_q), .in3(nand_1_out), .out(SQOUT), .sel(SQ_DUTY));

  // Notes on the sheet:
  //   W4003  SQUARE 0
  //   W4007  SQUARE 1
  //   W4000 SQUARE 0
  //   W4004 SQUARE 1
  //   not used
  //   INV3
  //   NAND1
  //   NOR10
  //   12.5%
  //   25%
  //   INV4
  //   75%
  //   50%
endmodule

// TRIANGLE CHANNEL
module TRIANGLE_CHANNEL (
  input  PHI1,
  input  nACLK,
  input  W400A,
  input  D0,
  input  D1,
  input  D2,
  input  D3,
  input  D4,
  input  D5,
  input  D6,
  input  D7,
  input  W4008,
  input  W400B,
  input  W401A,
  input  nLFO1,
  input  RES,
  input  NOTRI,
  input  LOCk,
  output [10:0] TRI_FREQ,
  output [7:0] TRI_LIN,
  output TRI0,
  output TRI1,
  output TRI2,
  output TRI3,
  output TRI_LC
);

  wire _5_out, triangle_frequency_down_counter_1_nfout, triangle_linear_down_counter_1_tco;

  TRIANGLE_FREQUENCY_DOWN_COUNTER triangle_frequency_down_counter_1 (
    .PHI1(PHI1), .W400A(W400A), .W400B(W400B), .RES(RES), .D0(D0), .D1(D1), .D2(D2), .D3(D3), .D4(D4),
    .D5(D5), .D6(D6), .D7(D7), .nFOUT(triangle_frequency_down_counter_1_nfout), .out_13(TRI_FREQ));
  TRIANGLE_LINEAR_DOWN_COUNTER triangle_linear_down_counter_1 (
    .nACLK(nACLK), .W4008(W4008), .W400B(W400B), .nLFO1(nLFO1), .RES(RES), .D0(D0), .D1(D1), .D2(D2),
    .D3(D3), .D4(D4), .D5(D5), .TCO(triangle_linear_down_counter_1_tco), .D6(D6), .D7(D7), .TRI_LC(TRI_LC),
    .TRI_LIN(TRI_LIN));
  nor _5 (_5_out, PHI1, triangle_frequency_down_counter_1_nfout, triangle_linear_down_counter_1_tco, NOTRI, LOCk);
  TRIANGLE_OUTPUT_COUNTER triangle_output_counter_1 (
    .PHI1(PHI1), .TTSTEP(_5_out), .RES(RES), .TRI0(TRI0), .TRI1(TRI1), .TRI2(TRI2), .TRI3(TRI3),
    .W401A(W401A), .D0(D0), .D1(D1), .D2(D2), .D3(D3), .D4(D4));
endmodule
// TRIANGLE FREQUENCY DOWN COUNTER
module TRIANGLE_FREQUENCY_DOWN_COUNTER (
  input  PHI1,
  input  RES,
  input  W400A,
  input  D0,
  input  D1,
  input  D2,
  input  D3,
  input  D4,
  input  D5,
  input  D6,
  input  D7,
  input  W400B,
  output [10:0] out_13,
  output nFOUT
);

  wire _1_out, _2_out, d_ff_12_q, d_ff_12_qn, d_ff_13_q, d_ff_13_qn, d_ff_14_q, d_ff_14_qn, d_ff_15_q,
       d_ff_15_qn, d_ff_16_q, d_ff_16_qn, d_ff_17_q, d_ff_17_qn, d_ff_18_q, d_ff_18_qn, d_ff_19_q,
       d_ff_19_qn, d_ff_20_q, d_ff_20_qn, d_ff_21_q, d_ff_21_qn, d_ff_22_q, d_ff_22_qn, d_ff_23_qn,
       d_ff_24_qn, d_ff_25_qn, d_ff_26_qn, d_ff_27_qn, d_ff_28_qn, d_ff_29_qn, d_ff_30_qn, d_ff_31_qn,
       d_ff_32_qn, d_ff_33_qn, demultiplexer_1_out0, demultiplexer_1_out1, demultiplexer_2_out0,
       demultiplexer_2_out1, demultiplexer_3_out0, demultiplexer_3_out1, demultiplexer_4_out0,
       demultiplexer_4_out1, demultiplexer_5_out0, demultiplexer_5_out1, demultiplexer_6_out0,
       demultiplexer_6_out1, demultiplexer_7_out0, demultiplexer_7_out1, demultiplexer_8_out0,
       demultiplexer_8_out1, demultiplexer_9_out0, demultiplexer_9_out1, demultiplexer_10_out0,
       demultiplexer_10_out1, demultiplexer_11_out0, demultiplexer_11_out1, nor_1_out, nor_2_out, nor_3_out,
       nor_4_out, nor_5_out, nor_6_out, nor_7_out, nor_8_out, nor_9_out, nor_10_out, nor_11_out, not_1_out,
       not_2_out, not_3_out, not_4_out, not_5_out, not_6_out, not_7_out, not_8_out, not_9_out, not_10_out,
       not_11_out, not_12_out, not_13_out, or_1_out, or_2_out, or_3_out, or_4_out, or_5_out, or_6_out,
       or_7_out, or_8_out, or_9_out, or_10_out, or_11_out, xor_1_out, xor_2_out, xor_3_out, xor_4_out,
       xor_5_out, xor_6_out, xor_7_out, xor_8_out, xor_9_out, xor_10_out, xor_11_out;

  not not_1 (not_1_out, PHI1);
  D_Flip_Flop #(.trigger("high")) d_ff_1 (
    .clk(not_1_out), .D(D0), .Q(out_13[0]), .en(W400A));  // open: Qn, preset, reset
  Demultiplexer #(.enable("false")) demultiplexer_1 (
    .out0(demultiplexer_1_out0), .out1(demultiplexer_1_out1), .in(_2_out), .sel(out_13[0]));
  D_Flip_Flop #(.trigger("high")) d_ff_2 (
    .clk(not_1_out), .D(D1), .Q(out_13[1]), .en(W400A));  // open: Qn, preset, reset
  Demultiplexer #(.enable("false")) demultiplexer_2 (
    .out0(demultiplexer_2_out0), .out1(demultiplexer_2_out1), .in(_2_out), .sel(out_13[1]));
  D_Flip_Flop #(.trigger("high")) d_ff_3 (
    .clk(not_1_out), .D(D2), .Q(out_13[2]), .en(W400A));  // open: Qn, preset, reset
  Demultiplexer #(.enable("false")) demultiplexer_3 (
    .out0(demultiplexer_3_out0), .out1(demultiplexer_3_out1), .in(_2_out), .sel(out_13[2]));
  D_Flip_Flop #(.trigger("high")) d_ff_4 (
    .clk(not_1_out), .D(D3), .Q(out_13[3]), .en(W400A));  // open: Qn, preset, reset
  Demultiplexer #(.enable("false")) demultiplexer_4 (
    .out0(demultiplexer_4_out0), .out1(demultiplexer_4_out1), .in(_2_out), .sel(out_13[3]));
  D_Flip_Flop #(.trigger("high")) d_ff_5 (
    .clk(not_1_out), .D(D4), .Q(out_13[4]), .en(W400A));  // open: Qn, preset, reset
  Demultiplexer #(.enable("false")) demultiplexer_5 (
    .out0(demultiplexer_5_out0), .out1(demultiplexer_5_out1), .in(_2_out), .sel(out_13[4]));
  D_Flip_Flop #(.trigger("high")) d_ff_6 (
    .clk(not_1_out), .D(D5), .Q(out_13[5]), .en(W400A));  // open: Qn, preset, reset
  Demultiplexer #(.enable("false")) demultiplexer_6 (
    .out0(demultiplexer_6_out0), .out1(demultiplexer_6_out1), .in(_2_out), .sel(out_13[5]));
  D_Flip_Flop #(.trigger("high")) d_ff_7 (
    .clk(not_1_out), .D(D6), .Q(out_13[6]), .en(W400A));  // open: Qn, preset, reset
  Demultiplexer #(.enable("false")) demultiplexer_7 (
    .out0(demultiplexer_7_out0), .out1(demultiplexer_7_out1), .in(_2_out), .sel(out_13[6]));
  D_Flip_Flop #(.trigger("high")) d_ff_8 (
    .clk(not_1_out), .D(D7), .Q(out_13[7]), .en(W400A));  // open: Qn, preset, reset
  Demultiplexer #(.enable("false")) demultiplexer_8 (
    .out0(demultiplexer_8_out0), .out1(demultiplexer_8_out1), .in(_2_out), .sel(out_13[7]));
  D_Flip_Flop #(.trigger("high")) d_ff_9 (
    .clk(not_1_out), .D(D0), .Q(out_13[8]), .en(W400B));  // open: Qn, preset, reset
  Demultiplexer #(.enable("false")) demultiplexer_9 (
    .out0(demultiplexer_9_out0), .out1(demultiplexer_9_out1), .in(_2_out), .sel(out_13[8]));
  D_Flip_Flop #(.trigger("high")) d_ff_10 (
    .clk(not_1_out), .D(D1), .Q(out_13[9]), .en(W400B));  // open: Qn, preset, reset
  Demultiplexer #(.enable("false")) demultiplexer_10 (
    .out0(demultiplexer_10_out0), .out1(demultiplexer_10_out1), .in(_2_out), .sel(out_13[9]));
  D_Flip_Flop #(.trigger("high")) d_ff_11 (
    .clk(not_1_out), .D(D2), .Q(out_13[10]), .en(W400B));  // open: Qn, preset, reset
  Demultiplexer #(.enable("false")) demultiplexer_11 (
    .out0(demultiplexer_11_out0), .out1(demultiplexer_11_out1), .in(_2_out), .sel(out_13[10]));
  or or_1 (or_1_out, RES, demultiplexer_1_out0);
  or or_2 (or_2_out, RES, demultiplexer_2_out0);
  or or_3 (or_3_out, RES, demultiplexer_3_out0);
  or or_4 (or_4_out, RES, demultiplexer_4_out0);
  or or_5 (or_5_out, RES, demultiplexer_5_out0);
  or or_6 (or_6_out, RES, demultiplexer_6_out0);
  or or_7 (or_7_out, RES, demultiplexer_7_out0);
  or or_8 (or_8_out, RES, demultiplexer_8_out0);
  or or_9 (or_9_out, RES, demultiplexer_9_out0);
  or or_10 (or_10_out, RES, demultiplexer_10_out0);
  or or_11 (or_11_out, RES, demultiplexer_11_out0);
  D_Flip_Flop #(.trigger("high")) d_ff_12 (
    .clk(_1_out), .D(d_ff_23_qn), .Q(d_ff_12_q), .Qn(d_ff_12_qn), .preset(demultiplexer_1_out1),
    .reset(or_1_out));  // open: en
  D_Flip_Flop #(.trigger("high")) d_ff_13 (
    .clk(_1_out), .D(d_ff_24_qn), .Q(d_ff_13_q), .Qn(d_ff_13_qn), .preset(demultiplexer_2_out1),
    .reset(or_2_out));  // open: en
  D_Flip_Flop #(.trigger("high")) d_ff_14 (
    .clk(_1_out), .D(d_ff_25_qn), .Q(d_ff_14_q), .Qn(d_ff_14_qn), .preset(demultiplexer_3_out1),
    .reset(or_3_out));  // open: en
  D_Flip_Flop #(.trigger("high")) d_ff_15 (
    .clk(_1_out), .D(d_ff_26_qn), .Q(d_ff_15_q), .Qn(d_ff_15_qn), .preset(demultiplexer_4_out1),
    .reset(or_4_out));  // open: en
  D_Flip_Flop #(.trigger("high")) d_ff_16 (
    .clk(_1_out), .D(d_ff_27_qn), .Q(d_ff_16_q), .Qn(d_ff_16_qn), .preset(demultiplexer_5_out1),
    .reset(or_5_out));  // open: en
  D_Flip_Flop #(.trigger("high")) d_ff_17 (
    .clk(_1_out), .D(d_ff_28_qn), .Q(d_ff_17_q), .Qn(d_ff_17_qn), .preset(demultiplexer_6_out1),
    .reset(or_6_out));  // open: en
  D_Flip_Flop #(.trigger("high")) d_ff_18 (
    .clk(_1_out), .D(d_ff_29_qn), .Q(d_ff_18_q), .Qn(d_ff_18_qn), .preset(demultiplexer_7_out1),
    .reset(or_7_out));  // open: en
  D_Flip_Flop #(.trigger("high")) d_ff_19 (
    .clk(_1_out), .D(d_ff_30_qn), .Q(d_ff_19_q), .Qn(d_ff_19_qn), .preset(demultiplexer_8_out1),
    .reset(or_8_out));  // open: en
  D_Flip_Flop #(.trigger("high")) d_ff_20 (
    .clk(_1_out), .D(d_ff_31_qn), .Q(d_ff_20_q), .Qn(d_ff_20_qn), .preset(demultiplexer_9_out1),
    .reset(or_9_out));  // open: en
  D_Flip_Flop #(.trigger("high")) d_ff_21 (
    .clk(_1_out), .D(d_ff_32_qn), .Q(d_ff_21_q), .Qn(d_ff_21_qn), .preset(demultiplexer_10_out1),
    .reset(or_10_out));  // open: en
  D_Flip_Flop #(.trigger("high")) d_ff_22 (
    .clk(_1_out), .D(d_ff_33_qn), .Q(d_ff_22_q), .Qn(d_ff_22_qn), .preset(demultiplexer_11_out1),
    .reset(or_11_out));  // open: en
  xor xor_1 (xor_1_out, 1'b1, d_ff_12_qn);
  not not_2 (not_2_out, 1'b1);
  nor nor_1 (nor_1_out, not_2_out, d_ff_12_q);
  xor xor_2 (xor_2_out, nor_1_out, d_ff_13_qn);
  not not_3 (not_3_out, nor_1_out);
  nor nor_2 (nor_2_out, not_3_out, d_ff_13_q);
  xor xor_3 (xor_3_out, nor_2_out, d_ff_14_qn);
  not not_4 (not_4_out, nor_2_out);
  nor nor_3 (nor_3_out, not_4_out, d_ff_14_q);
  xor xor_4 (xor_4_out, nor_3_out, d_ff_15_qn);
  not not_5 (not_5_out, nor_3_out);
  nor nor_4 (nor_4_out, not_5_out, d_ff_15_q);
  xor xor_5 (xor_5_out, nor_4_out, d_ff_16_qn);
  not not_6 (not_6_out, nor_4_out);
  nor nor_5 (nor_5_out, not_6_out, d_ff_16_q);
  xor xor_6 (xor_6_out, nor_5_out, d_ff_17_qn);
  not not_7 (not_7_out, nor_5_out);
  nor nor_6 (nor_6_out, not_7_out, d_ff_17_q);
  xor xor_7 (xor_7_out, nor_6_out, d_ff_18_qn);
  not not_8 (not_8_out, nor_6_out);
  nor nor_7 (nor_7_out, not_8_out, d_ff_18_q);
  xor xor_8 (xor_8_out, nor_7_out, d_ff_19_qn);
  not not_9 (not_9_out, nor_7_out);
  nor nor_8 (nor_8_out, not_9_out, d_ff_19_q);
  xor xor_9 (xor_9_out, nor_8_out, d_ff_20_qn);
  not not_10 (not_10_out, nor_8_out);
  nor nor_9 (nor_9_out, not_10_out, d_ff_20_q);
  xor xor_10 (xor_10_out, nor_9_out, d_ff_21_qn);
  not not_11 (not_11_out, nor_9_out);
  nor nor_10 (nor_10_out, not_11_out, d_ff_21_q);
  xor xor_11 (xor_11_out, nor_10_out, d_ff_22_qn);
  not not_12 (not_12_out, nor_10_out);
  nor nor_11 (nor_11_out, not_12_out, d_ff_22_q);
  nor _1 (_1_out, PHI1, not_13_out);
  nor _2 (_2_out, PHI1, nFOUT);
  D_Flip_Flop #(.trigger("high")) d_ff_23 (.clk(PHI1), .D(xor_1_out), .Qn(d_ff_23_qn));  // open: Q, preset, en, reset
  D_Flip_Flop #(.trigger("high")) d_ff_24 (.clk(PHI1), .D(xor_2_out), .Qn(d_ff_24_qn));  // open: Q, preset, en, reset
  D_Flip_Flop #(.trigger("high")) d_ff_25 (.clk(PHI1), .D(xor_3_out), .Qn(d_ff_25_qn));  // open: Q, preset, en, reset
  D_Flip_Flop #(.trigger("high")) d_ff_26 (.clk(PHI1), .D(xor_4_out), .Qn(d_ff_26_qn));  // open: Q, preset, en, reset
  D_Flip_Flop #(.trigger("high")) d_ff_27 (.clk(PHI1), .D(xor_5_out), .Qn(d_ff_27_qn));  // open: Q, preset, en, reset
  D_Flip_Flop #(.trigger("high")) d_ff_28 (.clk(PHI1), .D(xor_6_out), .Qn(d_ff_28_qn));  // open: Q, preset, en, reset
  D_Flip_Flop #(.trigger("high")) d_ff_29 (.clk(PHI1), .D(xor_7_out), .Qn(d_ff_29_qn));  // open: Q, preset, en, reset
  D_Flip_Flop #(.trigger("high")) d_ff_30 (.clk(PHI1), .D(xor_8_out), .Qn(d_ff_30_qn));  // open: Q, preset, en, reset
  D_Flip_Flop #(.trigger("high")) d_ff_31 (.clk(PHI1), .D(xor_9_out), .Qn(d_ff_31_qn));  // open: Q, preset, en, reset
  D_Flip_Flop #(.trigger("high")) d_ff_32 (.clk(PHI1), .D(xor_10_out), .Qn(d_ff_32_qn));  // open: Q, preset, en, reset
  D_Flip_Flop #(.trigger("high")) d_ff_33 (.clk(PHI1), .D(xor_11_out), .Qn(d_ff_33_qn));  // open: Q, preset, en, reset
  D_latch d_latch_1 (.EN(PHI1), .D(nor_11_out), .NOT_Q(nFOUT));  // open: Q
  not not_13 (not_13_out, nFOUT);

  // Notes on the sheet:
  //   TFSTEP
  //   TFLOAD
  //   4
  //   3
endmodule

// TRIANGLE LINEAR DOWN COUNTER
module TRIANGLE_LINEAR_DOWN_COUNTER (
  input  nACLK,
  input  RES,
  input  W4008,
  input  D0,
  input  D1,
  input  D2,
  input  D3,
  input  D4,
  input  D5,
  input  D6,
  input  D7,
  input  W400B,
  input  nLFO1,
  output [7:0] TRI_LIN,
  output TCO,
  output TRI_LC
);

  wire _8_out, _9_out, _11_out, _12_out, _13_out, d_ff_9_q, d_ff_9_qn, d_ff_10_q, d_ff_10_qn, d_ff_11_q,
       d_ff_11_qn, d_ff_12_q, d_ff_12_qn, d_ff_13_q, d_ff_13_qn, d_ff_14_q, d_ff_14_qn, d_ff_15_q,
       d_ff_15_qn, d_ff_16_qn, d_ff_17_qn, d_ff_18_qn, d_ff_19_qn, d_ff_20_qn, d_ff_21_qn, d_ff_22_qn,
       d_latch_1_q, d_latch_2_q, d_latch_3_not_q, demultiplexer_1_out0, demultiplexer_1_out1,
       demultiplexer_2_out0, demultiplexer_2_out1, demultiplexer_3_out0, demultiplexer_3_out1,
       demultiplexer_4_out0, demultiplexer_4_out1, demultiplexer_5_out0, demultiplexer_5_out1,
       demultiplexer_6_out0, demultiplexer_6_out1, demultiplexer_7_out0, demultiplexer_7_out1, nor_1_out,
       nor_2_out, nor_3_out, nor_4_out, nor_5_out, nor_6_out, not_1_out, not_2_out, not_3_out, not_4_out,
       not_5_out, not_6_out, not_7_out, not_8_out, not_9_out, or_1_out, or_2_out, or_3_out, or_4_out,
       or_5_out, or_6_out, or_7_out, xor_1_out, xor_2_out, xor_3_out, xor_4_out, xor_5_out, xor_6_out,
       xor_7_out;

  not not_1 (not_1_out, nACLK);
  D_Flip_Flop #(.trigger("high")) d_ff_1 (
    .clk(not_1_out), .D(D0), .Q(TRI_LIN[0]), .en(W4008));  // open: Qn, preset, reset
  D_Flip_Flop #(.trigger("high")) d_ff_2 (
    .clk(not_1_out), .D(D1), .Q(TRI_LIN[1]), .en(W4008));  // open: Qn, preset, reset
  D_Flip_Flop #(.trigger("high")) d_ff_3 (
    .clk(not_1_out), .D(D2), .Q(TRI_LIN[2]), .en(W4008));  // open: Qn, preset, reset
  D_Flip_Flop #(.trigger("high")) d_ff_4 (
    .clk(not_1_out), .D(D3), .Q(TRI_LIN[3]), .en(W4008));  // open: Qn, preset, reset
  D_Flip_Flop #(.trigger("high")) d_ff_5 (
    .clk(not_1_out), .D(D4), .Q(TRI_LIN[4]), .en(W4008));  // open: Qn, preset, reset
  D_Flip_Flop #(.trigger("high")) d_ff_6 (
    .clk(not_1_out), .D(D5), .Q(TRI_LIN[5]), .en(W4008));  // open: Qn, preset, reset
  D_Flip_Flop #(.trigger("high")) d_ff_7 (
    .clk(not_1_out), .D(D6), .Q(TRI_LIN[6]), .en(W4008));  // open: Qn, preset, reset
  D_Flip_Flop #(.trigger("high")) d_ff_8 (
    .clk(not_1_out), .D(D7), .Q(TRI_LIN[7]), .Qn(TRI_LC), .en(W4008));  // open: preset, reset
  Demultiplexer #(.enable("false")) demultiplexer_1 (
    .out0(demultiplexer_1_out0), .out1(demultiplexer_1_out1), .in(_8_out), .sel(TRI_LIN[0]));
  Demultiplexer #(.enable("false")) demultiplexer_2 (
    .out0(demultiplexer_2_out0), .out1(demultiplexer_2_out1), .in(_8_out), .sel(TRI_LIN[1]));
  Demultiplexer #(.enable("false")) demultiplexer_3 (
    .out0(demultiplexer_3_out0), .out1(demultiplexer_3_out1), .in(_8_out), .sel(TRI_LIN[2]));
  Demultiplexer #(.enable("false")) demultiplexer_4 (
    .out0(demultiplexer_4_out0), .out1(demultiplexer_4_out1), .in(_8_out), .sel(TRI_LIN[3]));
  Demultiplexer #(.enable("false")) demultiplexer_5 (
    .out0(demultiplexer_5_out0), .out1(demultiplexer_5_out1), .in(_8_out), .sel(TRI_LIN[4]));
  Demultiplexer #(.enable("false")) demultiplexer_6 (
    .out0(demultiplexer_6_out0), .out1(demultiplexer_6_out1), .in(_8_out), .sel(TRI_LIN[5]));
  Demultiplexer #(.enable("false")) demultiplexer_7 (
    .out0(demultiplexer_7_out0), .out1(demultiplexer_7_out1), .in(_8_out), .sel(TRI_LIN[6]));
  or or_1 (or_1_out, RES, demultiplexer_1_out0);
  or or_2 (or_2_out, RES, demultiplexer_2_out0);
  or or_3 (or_3_out, RES, demultiplexer_3_out0);
  or or_4 (or_4_out, RES, demultiplexer_4_out0);
  or or_5 (or_5_out, RES, demultiplexer_5_out0);
  or or_6 (or_6_out, RES, demultiplexer_6_out0);
  or or_7 (or_7_out, RES, demultiplexer_7_out0);
  nor _11 (_11_out, d_latch_1_q, TRI_LIN[7], nLFO1);
  D_Flip_Flop #(.trigger("high")) d_ff_9 (
    .clk(_9_out), .D(d_ff_16_qn), .Q(d_ff_9_q), .Qn(d_ff_9_qn), .preset(demultiplexer_1_out1),
    .reset(or_1_out));  // open: en
  D_Flip_Flop #(.trigger("high")) d_ff_10 (
    .clk(_9_out), .D(d_ff_17_qn), .Q(d_ff_10_q), .Qn(d_ff_10_qn), .preset(demultiplexer_2_out1),
    .reset(or_2_out));  // open: en
  D_Flip_Flop #(.trigger("high")) d_ff_11 (
    .clk(_9_out), .D(d_ff_18_qn), .Q(d_ff_11_q), .Qn(d_ff_11_qn), .preset(demultiplexer_3_out1),
    .reset(or_3_out));  // open: en
  D_Flip_Flop #(.trigger("high")) d_ff_12 (
    .clk(_9_out), .D(d_ff_19_qn), .Q(d_ff_12_q), .Qn(d_ff_12_qn), .preset(demultiplexer_4_out1),
    .reset(or_4_out));  // open: en
  D_Flip_Flop #(.trigger("high")) d_ff_13 (
    .clk(_9_out), .D(d_ff_20_qn), .Q(d_ff_13_q), .Qn(d_ff_13_qn), .preset(demultiplexer_5_out1),
    .reset(or_5_out));  // open: en
  D_Flip_Flop #(.trigger("high")) d_ff_14 (
    .clk(_9_out), .D(d_ff_21_qn), .Q(d_ff_14_q), .Qn(d_ff_14_qn), .preset(demultiplexer_6_out1),
    .reset(or_6_out));  // open: en
  D_Flip_Flop #(.trigger("high")) d_ff_15 (
    .clk(_9_out), .D(d_ff_22_qn), .Q(d_ff_15_q), .Qn(d_ff_15_qn), .preset(demultiplexer_7_out1),
    .reset(or_7_out));  // open: en
  nor _12 (_12_out, _11_out, _13_out);
  nor _13 (_13_out, _12_out, W400B);
  xor xor_1 (xor_1_out, 1'b1, d_ff_9_qn);
  not not_2 (not_2_out, 1'b1);
  nor nor_1 (nor_1_out, not_2_out, d_ff_9_q);
  xor xor_2 (xor_2_out, nor_1_out, d_ff_10_qn);
  not not_3 (not_3_out, nor_1_out);
  nor nor_2 (nor_2_out, not_3_out, d_ff_10_q);
  xor xor_3 (xor_3_out, nor_2_out, d_ff_11_qn);
  not not_4 (not_4_out, nor_2_out);
  nor nor_3 (nor_3_out, not_4_out, d_ff_11_q);
  xor xor_4 (xor_4_out, nor_3_out, d_ff_12_qn);
  not not_5 (not_5_out, nor_3_out);
  nor nor_4 (nor_4_out, not_5_out, d_ff_12_q);
  xor xor_5 (xor_5_out, nor_4_out, d_ff_13_qn);
  not not_6 (not_6_out, nor_4_out);
  nor nor_5 (nor_5_out, not_6_out, d_ff_13_q);
  xor xor_6 (xor_6_out, nor_5_out, d_ff_14_qn);
  not not_7 (not_7_out, nor_5_out);
  nor nor_6 (nor_6_out, not_7_out, d_ff_14_q);
  xor xor_7 (xor_7_out, nor_6_out, d_ff_15_qn);
  not not_8 (not_8_out, nor_6_out);
  nor nor_7 (TCO, not_8_out, d_ff_15_q);
  D_Flip_Flop #(.trigger("high")) d_ff_16 (.clk(nACLK), .D(xor_1_out), .Qn(d_ff_16_qn));  // open: Q, preset, en, reset
  D_Flip_Flop #(.trigger("high")) d_ff_17 (.clk(nACLK), .D(xor_2_out), .Qn(d_ff_17_qn));  // open: Q, preset, en, reset
  D_Flip_Flop #(.trigger("high")) d_ff_18 (.clk(nACLK), .D(xor_3_out), .Qn(d_ff_18_qn));  // open: Q, preset, en, reset
  D_Flip_Flop #(.trigger("high")) d_ff_19 (.clk(nACLK), .D(xor_4_out), .Qn(d_ff_19_qn));  // open: Q, preset, en, reset
  D_Flip_Flop #(.trigger("high")) d_ff_20 (.clk(nACLK), .D(xor_5_out), .Qn(d_ff_20_qn));  // open: Q, preset, en, reset
  D_Flip_Flop #(.trigger("high")) d_ff_21 (.clk(nACLK), .D(xor_6_out), .Qn(d_ff_21_qn));  // open: Q, preset, en, reset
  D_Flip_Flop #(.trigger("high")) d_ff_22 (.clk(nACLK), .D(xor_7_out), .Qn(d_ff_22_qn));  // open: Q, preset, en, reset
  D_latch d_latch_1 (.EN(nACLK), .D(_13_out), .Q(d_latch_1_q));  // open: NOT_Q
  D_latch d_latch_2 (.EN(nACLK), .D(TCO), .Q(d_latch_2_q));  // open: NOT_Q
  not not_9 (not_9_out, d_latch_3_not_q);
  D_latch d_latch_3 (.EN(nACLK), .D(_12_out), .NOT_Q(d_latch_3_not_q));  // open: Q
  nor _9 (_9_out, d_latch_2_q, not_9_out, nLFO1);
  nor _8 (_8_out, nLFO1, d_latch_3_not_q);

  // Notes on the sheet:
  //   10
  //   R
  //   S
  //   TRELOAD
  //   Q
  //   RELOAD  FF
  //   /Q
  //   TCO
  //   TCO
  //   11
  //   RELOAD LATCH 1
  //   14
  //   TCO LATCH
  //   6,7
  //   RELOAD LATCH 2
  //   TSTEP
  //   TLOAD
endmodule

// TRIANGLE OUTPUT COUNTER
module TRIANGLE_OUTPUT_COUNTER (
  input  PHI1,
  input  TTSTEP,
  input  RES,
  input  D0,
  input  W401A,
  input  D1,
  input  D2,
  input  D3,
  input  D4,
  output TRI0,
  output TRI1,
  output TRI2,
  output TRI3
);

  wire d_ff_1_q, d_ff_1_qn, d_ff_2_q, d_ff_2_qn, d_ff_3_q, d_ff_3_qn, d_ff_4_q, d_ff_4_qn, d_ff_5_q,
       d_ff_5_qn, d_ff_6_qn, d_ff_7_qn, d_ff_8_qn, d_ff_9_qn, d_ff_10_qn, demultiplexer_1_out0,
       demultiplexer_1_out1, demultiplexer_2_out0, demultiplexer_2_out1, demultiplexer_3_out0,
       demultiplexer_3_out1, demultiplexer_4_out0, demultiplexer_4_out1, demultiplexer_5_out0,
       demultiplexer_5_out1, nor_1_out, nor_2_out, nor_3_out, nor_4_out, nor_5_out, not_1_out, not_2_out,
       not_3_out, not_4_out, not_5_out, or_1_out, or_2_out, or_3_out, or_4_out, or_5_out, xor_1_out,
       xor_2_out, xor_3_out, xor_4_out, xor_5_out;

  Demultiplexer #(.enable("false")) demultiplexer_1 (
    .out0(demultiplexer_1_out0), .out1(demultiplexer_1_out1), .in(W401A), .sel(D0));
  Demultiplexer #(.enable("false")) demultiplexer_2 (
    .out0(demultiplexer_2_out0), .out1(demultiplexer_2_out1), .in(W401A), .sel(D1));
  Demultiplexer #(.enable("false")) demultiplexer_3 (
    .out0(demultiplexer_3_out0), .out1(demultiplexer_3_out1), .in(W401A), .sel(D2));
  Demultiplexer #(.enable("false")) demultiplexer_4 (
    .out0(demultiplexer_4_out0), .out1(demultiplexer_4_out1), .in(W401A), .sel(D3));
  Demultiplexer #(.enable("false")) demultiplexer_5 (
    .out0(demultiplexer_5_out0), .out1(demultiplexer_5_out1), .in(W401A), .sel(D4));
  or or_1 (or_1_out, RES, demultiplexer_1_out0);
  or or_2 (or_2_out, RES, demultiplexer_2_out0);
  or or_3 (or_3_out, RES, demultiplexer_3_out0);
  or or_4 (or_4_out, RES, demultiplexer_4_out0);
  or or_5 (or_5_out, RES, demultiplexer_5_out0);
  D_Flip_Flop #(.trigger("high")) d_ff_1 (
    .clk(TTSTEP), .D(d_ff_6_qn), .Q(d_ff_1_q), .Qn(d_ff_1_qn), .preset(demultiplexer_1_out1), .reset(or_1_out));  // open: en
  D_Flip_Flop #(.trigger("high")) d_ff_2 (
    .clk(TTSTEP), .D(d_ff_7_qn), .Q(d_ff_2_q), .Qn(d_ff_2_qn), .preset(demultiplexer_2_out1), .reset(or_2_out));  // open: en
  D_Flip_Flop #(.trigger("high")) d_ff_3 (
    .clk(TTSTEP), .D(d_ff_8_qn), .Q(d_ff_3_q), .Qn(d_ff_3_qn), .preset(demultiplexer_3_out1), .reset(or_3_out));  // open: en
  D_Flip_Flop #(.trigger("high")) d_ff_4 (
    .clk(TTSTEP), .D(d_ff_9_qn), .Q(d_ff_4_q), .Qn(d_ff_4_qn), .preset(demultiplexer_4_out1), .reset(or_4_out));  // open: en
  D_Flip_Flop #(.trigger("high")) d_ff_5 (
    .clk(TTSTEP), .D(d_ff_10_qn), .Q(d_ff_5_q), .Qn(d_ff_5_qn), .preset(demultiplexer_5_out1),
    .reset(or_5_out));  // open: en
  not not_1 (not_1_out, 1'b1);
  not not_2 (not_2_out, nor_1_out);
  not not_3 (not_3_out, nor_2_out);
  not not_4 (not_4_out, nor_3_out);
  not not_5 (not_5_out, nor_4_out);
  xor xor_1 (xor_1_out, 1'b1, d_ff_1_qn);
  nor nor_1 (nor_1_out, not_1_out, d_ff_1_qn);
  xor xor_2 (xor_2_out, nor_1_out, d_ff_2_qn);
  nor nor_2 (nor_2_out, not_2_out, d_ff_2_qn);
  xor xor_3 (xor_3_out, nor_2_out, d_ff_3_qn);
  nor nor_3 (nor_3_out, not_3_out, d_ff_3_qn);
  xor xor_4 (xor_4_out, nor_3_out, d_ff_4_qn);
  nor nor_4 (nor_4_out, not_4_out, d_ff_4_qn);
  xor xor_5 (xor_5_out, nor_4_out, d_ff_5_qn);
  nor nor_5 (nor_5_out, not_5_out, d_ff_5_qn);
  D_Flip_Flop #(.trigger("high")) d_ff_6 (.clk(PHI1), .D(xor_1_out), .Qn(d_ff_6_qn));  // open: Q, preset, en, reset
  D_Flip_Flop #(.trigger("high")) d_ff_7 (.clk(PHI1), .D(xor_2_out), .Qn(d_ff_7_qn));  // open: Q, preset, en, reset
  D_Flip_Flop #(.trigger("high")) d_ff_8 (.clk(PHI1), .D(xor_3_out), .Qn(d_ff_8_qn));  // open: Q, preset, en, reset
  D_Flip_Flop #(.trigger("high")) d_ff_9 (.clk(PHI1), .D(xor_4_out), .Qn(d_ff_9_qn));  // open: Q, preset, en, reset
  D_Flip_Flop #(.trigger("high")) d_ff_10 (.clk(PHI1), .D(xor_5_out), .Qn(d_ff_10_qn));  // open: Q, preset, en, reset
  xnor xnor_1 (TRI0, d_ff_1_q, d_ff_5_q);
  xnor xnor_2 (TRI1, d_ff_2_q, d_ff_5_q);
  xnor xnor_3 (TRI2, d_ff_3_q, d_ff_5_q);
  xnor xnor_4 (TRI3, d_ff_4_q, d_ff_5_q);

  // Notes on the sheet:
  //   not used
endmodule

// NOISE CHANNEL
module NOISE_CHANNEL (
  input  ACLK,
  input  nACLK,
  input  D0,
  input  D1,
  input  D2,
  input  D3,
  input  D4,
  input  D5,
  input  D7,
  input  NORND,
  input  LOCK,
  input  W400E,
  input  W400C,
  input  W400F,
  input  Res,
  input  nLFO1,
  output [3:0] N_FREQ,
  output RMODE,
  output RND0,
  output [5:0] N_ENV,
  output RND1,
  output RND2,
  output RND3,
  output nRND_LC
);

  wire noise_frequency_lfsr_1_rstep, random_lfsr_1_rndout;

  NOISE_FREQUENCY_LFSR noise_frequency_lfsr_1 (
    .nACLK(nACLK), .ACLK(ACLK), .RES(Res), .D0(D0), .D1(D1), .D2(D2), .D3(D3),
    .RSTEP(noise_frequency_lfsr_1_rstep), .W400E(W400E), .N_FREQ(N_FREQ));
  RANDOM_LFSR random_lfsr_1 (
    .RSTEP(noise_frequency_lfsr_1_rstep), .W400E(W400E), .D7(D7), .NORND(NORND),
    .RNDOUT(random_lfsr_1_rndout), .LOCK(LOCK), .nACLK(nACLK), .out_8(RMODE));
  ENVELOPE_GENERATOR envelope_generator_1 (
    .nACLK(nACLK), .W400_0__4__C(W400C), .W400_3__7__F(W400F), .D0(D0), .D1(D1), .D2(D2), .D3(D3), .D4(D4),
    .D5(D5), .nLFO1(nLFO1), .RES(Res), .V0(RND0), .V1(RND1), .V2(RND2), .V3(RND3), .nCH_LC(nRND_LC),
    .CH_IN(random_lfsr_1_rndout), .ENV(N_ENV));
endmodule

// NOISE FREQUENCY LFSR
module NOISE_FREQUENCY_LFSR (
  input  nACLK,
  input  D0,
  input  D1,
  input  D2,
  input  D3,
  input  W400E,
  input  ACLK,
  input  RES,
  output [3:0] N_FREQ,
  output RSTEP
);

  wire _9_out, _11_out, _14_out, _15_2_out, _15_out, _16_out, d_ff_5_qn, d_ff_6_qn, d_ff_7_qn, d_ff_8_qn,
       d_ff_9_qn, d_ff_10_qn, d_ff_11_qn, d_ff_12_qn, d_ff_13_qn, d_ff_14_qn, d_ff_15_qn, d_latch_1_not_q,
       d_latch_2_not_q, d_latch_3_not_q, d_latch_4_not_q, d_latch_5_not_q, d_latch_6_not_q, d_latch_7_not_q,
       d_latch_8_not_q, d_latch_9_not_q, d_latch_10_not_q, d_latch_11_not_q, demultiplexer_1_out0,
       demultiplexer_1_out1, demultiplexer_2_out0, demultiplexer_2_out1, demultiplexer_3_out0,
       demultiplexer_3_out1, demultiplexer_4_out0, demultiplexer_4_out1, demultiplexer_5_out0,
       demultiplexer_5_out1, demultiplexer_6_out0, demultiplexer_6_out1, demultiplexer_7_out0,
       demultiplexer_7_out1, demultiplexer_8_out0, demultiplexer_8_out1, demultiplexer_9_out0,
       demultiplexer_9_out1, demultiplexer_10_out0, demultiplexer_10_out1, demultiplexer_11_out0,
       demultiplexer_11_out1, demultiplexer_12_out0, demultiplexer_12_out1, noise_table_1_nnf0,
       noise_table_1_nnf1, noise_table_1_nnf2, noise_table_1_nnf3, noise_table_1_nnf4, noise_table_1_nnf5,
       noise_table_1_nnf6, noise_table_1_nnf7, noise_table_1_nnf8, noise_table_1_nnf9, noise_table_1_nnf10,
       not_1_out, not_2_out, not_3_out, not_4_out, not_5_out;

  not not_1 (not_1_out, nACLK);
  D_Flip_Flop #(.trigger("high")) d_ff_1 (
    .clk(not_1_out), .D(D0), .Q(N_FREQ[0]), .en(W400E), .reset(RES));  // open: Qn, preset
  D_Flip_Flop #(.trigger("high")) d_ff_2 (
    .clk(not_1_out), .D(D1), .Q(N_FREQ[1]), .en(W400E), .reset(RES));  // open: Qn, preset
  D_Flip_Flop #(.trigger("high")) d_ff_3 (
    .clk(not_1_out), .D(D2), .Q(N_FREQ[2]), .en(W400E), .reset(RES));  // open: Qn, preset
  D_Flip_Flop #(.trigger("high")) d_ff_4 (
    .clk(not_1_out), .D(D3), .Q(N_FREQ[3]), .en(W400E), .reset(RES));  // open: Qn, preset
  not not_2 (not_2_out, not_3_out);
  not not_3 (not_3_out, ACLK);
  NOISE_TABLE noise_table_1 (
    .NNF0(noise_table_1_nnf0), .NNF1(noise_table_1_nnf1), .NNF2(noise_table_1_nnf2),
    .NNF3(noise_table_1_nnf3), .NNF4(noise_table_1_nnf4), .NNF5(noise_table_1_nnf5),
    .NNF6(noise_table_1_nnf6), .NNF7(noise_table_1_nnf7), .NNF8(noise_table_1_nnf8),
    .NNF9(noise_table_1_nnf9), .NNF10(noise_table_1_nnf10), .NF3(N_FREQ[3]), .NF2(N_FREQ[2]),
    .NF1(N_FREQ[1]), .NF0(N_FREQ[0]));
  not not_4 (not_4_out, _9_out);
  nor _11 (_11_out, not_2_out, _9_out);
  nor _12 (RSTEP, not_4_out, not_2_out);
  Demultiplexer #(.enable("false")) demultiplexer_1 (
    .out0(demultiplexer_1_out0), .out1(demultiplexer_1_out1), .in(RSTEP), .sel(noise_table_1_nnf10));
  Demultiplexer #(.enable("false")) demultiplexer_2 (
    .out0(demultiplexer_2_out0), .out1(demultiplexer_2_out1), .in(RSTEP), .sel(noise_table_1_nnf9));
  Demultiplexer #(.enable("false")) demultiplexer_3 (
    .out0(demultiplexer_3_out0), .out1(demultiplexer_3_out1), .in(RSTEP), .sel(noise_table_1_nnf8));
  Demultiplexer #(.enable("false")) demultiplexer_4 (
    .out0(demultiplexer_4_out0), .out1(demultiplexer_4_out1), .in(RSTEP), .sel(noise_table_1_nnf7));
  Demultiplexer #(.enable("false")) demultiplexer_5 (
    .out0(demultiplexer_5_out0), .out1(demultiplexer_5_out1), .in(RSTEP), .sel(noise_table_1_nnf6));
  Demultiplexer #(.enable("false")) demultiplexer_6 (
    .out0(demultiplexer_6_out0), .out1(demultiplexer_6_out1), .in(RSTEP), .sel(noise_table_1_nnf5));
  Demultiplexer #(.enable("false")) demultiplexer_7 (
    .out0(demultiplexer_7_out0), .out1(demultiplexer_7_out1), .in(RSTEP), .sel(noise_table_1_nnf4));
  Demultiplexer #(.enable("false")) demultiplexer_8 (
    .out0(demultiplexer_8_out0), .out1(demultiplexer_8_out1), .in(RSTEP), .sel(noise_table_1_nnf3));
  Demultiplexer #(.enable("false")) demultiplexer_9 (
    .out0(demultiplexer_9_out0), .out1(demultiplexer_9_out1), .in(RSTEP), .sel(noise_table_1_nnf2));
  Demultiplexer #(.enable("false")) demultiplexer_10 (
    .out0(demultiplexer_10_out0), .out1(demultiplexer_10_out1), .in(RSTEP), .sel(noise_table_1_nnf1));
  Demultiplexer #(.enable("false")) demultiplexer_11 (
    .out0(demultiplexer_11_out0), .out1(demultiplexer_11_out1), .in(RSTEP), .sel(noise_table_1_nnf0));
  nor _9 (_9_out, not_5_out, RES);
  D_Flip_Flop #(.trigger("high")) d_ff_5 (
    .clk(_11_out), .D(_15_2_out), .Qn(d_ff_5_qn), .preset(demultiplexer_1_out1), .reset(demultiplexer_1_out0));  // open: Q, en
  D_Flip_Flop #(.trigger("high")) d_ff_6 (
    .clk(_11_out), .D(d_latch_1_not_q), .Qn(d_ff_6_qn), .preset(demultiplexer_2_out1),
    .reset(demultiplexer_2_out0));  // open: Q, en
  D_Flip_Flop #(.trigger("high")) d_ff_7 (
    .clk(_11_out), .D(d_latch_2_not_q), .Qn(d_ff_7_qn), .preset(demultiplexer_3_out1),
    .reset(demultiplexer_3_out0));  // open: Q, en
  D_Flip_Flop #(.trigger("high")) d_ff_8 (
    .clk(_11_out), .D(d_latch_3_not_q), .Qn(d_ff_8_qn), .preset(demultiplexer_4_out1),
    .reset(demultiplexer_4_out0));  // open: Q, en
  D_Flip_Flop #(.trigger("high")) d_ff_9 (
    .clk(_11_out), .D(d_latch_4_not_q), .Qn(d_ff_9_qn), .preset(demultiplexer_5_out1),
    .reset(demultiplexer_5_out0));  // open: Q, en
  D_Flip_Flop #(.trigger("high")) d_ff_10 (
    .clk(_11_out), .D(d_latch_5_not_q), .Qn(d_ff_10_qn), .preset(demultiplexer_6_out1),
    .reset(demultiplexer_6_out0));  // open: Q, en
  D_Flip_Flop #(.trigger("high")) d_ff_11 (
    .clk(_11_out), .D(d_latch_6_not_q), .Qn(d_ff_11_qn), .preset(demultiplexer_7_out1),
    .reset(demultiplexer_7_out0));  // open: Q, en
  D_Flip_Flop #(.trigger("high")) d_ff_12 (
    .clk(_11_out), .D(d_latch_7_not_q), .Qn(d_ff_12_qn), .preset(demultiplexer_8_out1),
    .reset(demultiplexer_8_out0));  // open: Q, en
  D_Flip_Flop #(.trigger("high")) d_ff_13 (
    .clk(_11_out), .D(d_latch_8_not_q), .Qn(d_ff_13_qn), .preset(demultiplexer_9_out1),
    .reset(demultiplexer_9_out0));  // open: Q, en
  D_Flip_Flop #(.trigger("high")) d_ff_14 (
    .clk(_11_out), .D(d_latch_9_not_q), .Qn(d_ff_14_qn), .preset(demultiplexer_10_out1),
    .reset(demultiplexer_10_out0));  // open: Q, en
  D_Flip_Flop #(.trigger("high")) d_ff_15 (
    .clk(_11_out), .D(d_latch_10_not_q), .Qn(d_ff_15_qn), .preset(demultiplexer_11_out1),
    .reset(demultiplexer_11_out0));  // open: Q, en
  not not_5 (not_5_out, demultiplexer_12_out1);
  D_latch d_latch_1 (.EN(nACLK), .D(d_ff_5_qn), .NOT_Q(d_latch_1_not_q));  // open: Q
  D_latch d_latch_2 (.EN(nACLK), .D(d_ff_6_qn), .NOT_Q(d_latch_2_not_q));  // open: Q
  D_latch d_latch_3 (.EN(nACLK), .D(d_ff_7_qn), .NOT_Q(d_latch_3_not_q));  // open: Q
  D_latch d_latch_4 (.EN(nACLK), .D(d_ff_8_qn), .NOT_Q(d_latch_4_not_q));  // open: Q
  D_latch d_latch_5 (.EN(nACLK), .D(d_ff_9_qn), .NOT_Q(d_latch_5_not_q));  // open: Q
  D_latch d_latch_6 (.EN(nACLK), .D(d_ff_10_qn), .NOT_Q(d_latch_6_not_q));  // open: Q
  D_latch d_latch_7 (.EN(nACLK), .D(d_ff_11_qn), .NOT_Q(d_latch_7_not_q));  // open: Q
  D_latch d_latch_8 (.EN(nACLK), .D(d_ff_12_qn), .NOT_Q(d_latch_8_not_q));  // open: Q
  D_latch d_latch_9 (.EN(nACLK), .D(d_ff_13_qn), .NOT_Q(d_latch_9_not_q));  // open: Q
  D_latch d_latch_10 (.EN(nACLK), .D(d_ff_14_qn), .NOT_Q(d_latch_10_not_q));  // open: Q
  D_latch d_latch_11 (.EN(nACLK), .D(d_ff_15_qn), .NOT_Q(d_latch_11_not_q));  // open: Q
  and _15 (_15_out, d_latch_9_not_q, d_latch_11_not_q);
  nor _16 (_16_out, d_latch_1_not_q, d_latch_2_not_q, d_latch_3_not_q, d_latch_4_not_q, d_latch_5_not_q, d_latch_6_not_q, d_latch_7_not_q, d_latch_8_not_q, d_latch_9_not_q, d_latch_10_not_q);
  nor _14 (_14_out, d_latch_9_not_q, demultiplexer_12_out0, d_latch_11_not_q);
  Demultiplexer #(.disabled(0), .enable("false")) demultiplexer_12 (
    .out0(demultiplexer_12_out0), .out1(demultiplexer_12_out1), .in(_16_out), .sel(d_latch_11_not_q));
  nor _15_2 (_15_2_out, _14_out, RES, _15_out);

  // Notes on the sheet:
  //   10
  //   8
  //   13
  //   NFSTEP
  //   NFLOAD
  //   17
endmodule

// NOISE TABLE
module NOISE_TABLE (
  input  NF0,
  input  NF1,
  input  NF2,
  input  NF3,
  output NNF0,
  output NNF1,
  output NNF2,
  output NNF3,
  output NNF4,
  output NNF5,
  output NNF6,
  output NNF7,
  output NNF8,
  output NNF9,
  output NNF10
);

  Multiplexer #(.select(4), .width(11), .disabled(0), .enable("false")) multiplexer_1 (
    .in0(11'h2), .in1(11'ha), .in2(11'haa), .in3(11'h2bb), .in4(11'h139), .in5(11'h173), .in6(11'h63),
    .in7(11'h67), .in8(11'h1a9), .in9(11'h106), .in10(11'h227), .in11(11'h62), .in12(11'h642),
    .in13(11'h20f), .in14(11'h300), .in15(11'h140),
    .out({NNF10, NNF9, NNF8, NNF7, NNF6, NNF5, NNF4, NNF3, NNF2, NNF1, NNF0}), .sel({NF3, NF2, NF1, NF0}));

  // Notes on the sheet:
  //   NTSC
  //   PAL
  //   NTSC
endmodule

// RANDOM LFSR
module RANDOM_LFSR (
  input  nACLK,
  input  RSTEP,
  input  D7,
  input  W400E,
  input  NORND,
  input  LOCK,
  output RNDOUT,
  output out_8
);

  wire _2_2_out, _2_out, _3_out, _5_out, _6_out, d_ff_1_qn, d_ff_2_qn, d_ff_3_qn, d_ff_4_qn, d_ff_5_qn,
       d_ff_6_qn, d_ff_7_qn, d_ff_8_qn, d_ff_9_qn, d_ff_10_qn, d_ff_11_qn, d_ff_12_qn, d_ff_13_qn,
       d_ff_14_qn, d_ff_15_qn, d_latch_1_not_q, d_latch_2_not_q, d_latch_3_not_q, d_latch_4_not_q,
       d_latch_5_not_q, d_latch_6_not_q, d_latch_7_not_q, d_latch_8_not_q, d_latch_9_not_q, d_latch_10_not_q,
       d_latch_11_not_q, d_latch_12_not_q, d_latch_13_not_q, d_latch_14_not_q, d_latch_15_not_q,
       multiplexer_1_out, not_1_out;

  D_Flip_Flop #(.trigger("high")) d_ff_1 (.clk(RSTEP), .D(_2_2_out), .Qn(d_ff_1_qn));  // open: Q, preset, en, reset
  D_Flip_Flop #(.trigger("high")) d_ff_2 (
    .clk(RSTEP), .D(d_latch_1_not_q), .Qn(d_ff_2_qn));  // open: Q, preset, en, reset
  D_Flip_Flop #(.trigger("high")) d_ff_3 (
    .clk(RSTEP), .D(d_latch_2_not_q), .Qn(d_ff_3_qn));  // open: Q, preset, en, reset
  D_Flip_Flop #(.trigger("high")) d_ff_4 (
    .clk(RSTEP), .D(d_latch_3_not_q), .Qn(d_ff_4_qn));  // open: Q, preset, en, reset
  D_Flip_Flop #(.trigger("high")) d_ff_5 (
    .clk(RSTEP), .D(d_latch_4_not_q), .Qn(d_ff_5_qn));  // open: Q, preset, en, reset
  D_Flip_Flop #(.trigger("high")) d_ff_6 (
    .clk(RSTEP), .D(d_latch_5_not_q), .Qn(d_ff_6_qn));  // open: Q, preset, en, reset
  D_Flip_Flop #(.trigger("high")) d_ff_7 (
    .clk(RSTEP), .D(d_latch_6_not_q), .Qn(d_ff_7_qn));  // open: Q, preset, en, reset
  D_Flip_Flop #(.trigger("high")) d_ff_8 (
    .clk(RSTEP), .D(d_latch_7_not_q), .Qn(d_ff_8_qn));  // open: Q, preset, en, reset
  D_Flip_Flop #(.trigger("high")) d_ff_9 (
    .clk(RSTEP), .D(d_latch_8_not_q), .Qn(d_ff_9_qn));  // open: Q, preset, en, reset
  D_Flip_Flop #(.trigger("high")) d_ff_10 (
    .clk(RSTEP), .D(d_latch_9_not_q), .Qn(d_ff_10_qn));  // open: Q, preset, en, reset
  D_Flip_Flop #(.trigger("high")) d_ff_11 (
    .clk(RSTEP), .D(d_latch_10_not_q), .Qn(d_ff_11_qn));  // open: Q, preset, en, reset
  D_Flip_Flop #(.trigger("high")) d_ff_12 (
    .clk(RSTEP), .D(d_latch_11_not_q), .Qn(d_ff_12_qn));  // open: Q, preset, en, reset
  D_Flip_Flop #(.trigger("high")) d_ff_13 (
    .clk(RSTEP), .D(d_latch_12_not_q), .Qn(d_ff_13_qn));  // open: Q, preset, en, reset
  D_Flip_Flop #(.trigger("high")) d_ff_14 (
    .clk(RSTEP), .D(d_latch_13_not_q), .Qn(d_ff_14_qn));  // open: Q, preset, en, reset
  D_Flip_Flop #(.trigger("high")) d_ff_15 (
    .clk(RSTEP), .D(d_latch_14_not_q), .Qn(d_ff_15_qn));  // open: Q, preset, en, reset
  not not_1 (not_1_out, nACLK);
  D_latch d_latch_1 (.EN(nACLK), .D(d_ff_1_qn), .NOT_Q(d_latch_1_not_q));  // open: Q
  D_latch d_latch_2 (.EN(nACLK), .D(d_ff_2_qn), .NOT_Q(d_latch_2_not_q));  // open: Q
  D_latch d_latch_3 (.EN(nACLK), .D(d_ff_3_qn), .NOT_Q(d_latch_3_not_q));  // open: Q
  D_latch d_latch_4 (.EN(nACLK), .D(d_ff_4_qn), .NOT_Q(d_latch_4_not_q));  // open: Q
  D_latch d_latch_5 (.EN(nACLK), .D(d_ff_5_qn), .NOT_Q(d_latch_5_not_q));  // open: Q
  D_latch d_latch_6 (.EN(nACLK), .D(d_ff_6_qn), .NOT_Q(d_latch_6_not_q));  // open: Q
  D_latch d_latch_7 (.EN(nACLK), .D(d_ff_7_qn), .NOT_Q(d_latch_7_not_q));  // open: Q
  D_latch d_latch_8 (.EN(nACLK), .D(d_ff_8_qn), .NOT_Q(d_latch_8_not_q));  // open: Q
  D_latch d_latch_9 (.EN(nACLK), .D(d_ff_9_qn), .NOT_Q(d_latch_9_not_q));  // open: Q
  D_latch d_latch_10 (.EN(nACLK), .D(d_ff_10_qn), .NOT_Q(d_latch_10_not_q));  // open: Q
  D_latch d_latch_11 (.EN(nACLK), .D(d_ff_11_qn), .NOT_Q(d_latch_11_not_q));  // open: Q
  D_latch d_latch_12 (.EN(nACLK), .D(d_ff_12_qn), .NOT_Q(d_latch_12_not_q));  // open: Q
  D_latch d_latch_13 (.EN(nACLK), .D(d_ff_13_qn), .NOT_Q(d_latch_13_not_q));  // open: Q
  D_latch d_latch_14 (.EN(nACLK), .D(d_ff_14_qn), .NOT_Q(d_latch_14_not_q));  // open: Q
  D_latch d_latch_15 (.EN(nACLK), .D(d_ff_15_qn), .NOT_Q(d_latch_15_not_q));  // open: Q
  D_Flip_Flop #(.trigger("high")) d_ff_16 (.clk(not_1_out), .D(D7), .Q(out_8), .en(W400E));  // open: Qn, preset, reset
  Multiplexer #(.enable("false")) multiplexer_1 (
    .in0(d_latch_14_not_q), .in1(d_latch_9_not_q), .out(multiplexer_1_out), .sel(out_8));
  nor _5 (_5_out, d_latch_1_not_q, d_latch_2_not_q, d_latch_3_not_q, d_latch_4_not_q, d_latch_5_not_q, d_latch_6_not_q, d_latch_7_not_q, d_latch_8_not_q, d_latch_9_not_q, d_latch_10_not_q, d_latch_11_not_q, d_latch_12_not_q, d_latch_13_not_q, d_latch_14_not_q, d_latch_15_not_q);
  nor _3 (_3_out, d_latch_15_not_q, _5_out, multiplexer_1_out);
  and _2 (_2_out, multiplexer_1_out, d_latch_15_not_q);
  nor _6 (_6_out, d_latch_15_not_q, NORND);
  nor _2_2 (_2_2_out, _3_out, LOCK, _2_out);
  nor _7 (RNDOUT, _6_out, LOCK);

  // Notes on the sheet:
  //   DFF1
  //   R8
  //   R13
  //   R14
  //   4
endmodule

// DPCM CHANNEL
module DPCM_CHANNEL (
  input  PHI1,
  input  ACLK,
  input  nACLK,
  input  W4010,
  input  D0,
  input  D1,
  input  D2,
  input  D3,
  input  D4,
  input  D5,
  input  D6,
  input  D7,
  input  W4015,
  input  nR4015,
  input  LOCK,
  input  R_W,
  input  W4013,
  input  Res,
  input  W4011,
  input  W4012,
  output [3:0] DMC_F,
  output DMC_LOOP,
  output DMC_ENIRQ,
  output DMC_EN,
  output D4_2,
  output D7_2,
  output DMCINT,
  output RUNDMC,
  output DMCRDY,
  output nDMC_AB,
  output [7:0] SAMPLE_LENGTH,
  output DMC0,
  output DMC1,
  output DMC2,
  output DMC3,
  output DMC4,
  output DMC5,
  output DMC6,
  output [7:0] SAMPLE_ADR,
  output [7:0] SAMPLE_BUF,
  output DMCA0,
  output DMCA1,
  output DMCA2,
  output DMCA3,
  output DMCA4,
  output DMCA5,
  output DMCA6,
  output DMCA7,
  output DMCA8,
  output DMCA9,
  output DMCA10,
  output DMCA11,
  output DMCA12,
  output DMCA13,
  output DMCA14
);

  wire dpcm_control_1_bload, dpcm_control_1_bstep, dpcm_control_1_dsload, dpcm_control_1_dsstep,
       dpcm_control_1_dstep, dpcm_control_1_nstep, dpcm_control_1_pcm, dpcm_frequency_lfsr_1_dfload,
       dpcm_output_counter_1_dout, DPCM_SAMPLE_BIT_COUNTER_nnout, dpcm_sample_length_down_counter_1_sout,
       dpcm_sample_shift_register_1_nbout, nACLK2;

  not not_1 (nACLK2, ACLK);
  DPCM_FREQUENCY_LFSR dpcm_frequency_lfsr_1 (
    .nACLK(nACLK), .Res(Res), .D0(D0), .D1(D1), .D2(D2), .D3(D3), .DFLOAD(dpcm_frequency_lfsr_1_dfload),
    .nACLK2(nACLK2), .W4010(W4010), .DMC_F(DMC_F));
  DPCM_SAMPLE_BIT_COUNTER DPCM_SAMPLE_BIT_COUNTER (
    .nACLK(nACLK), .RES(Res), .NSTEP(dpcm_control_1_nstep), .nNOUT(DPCM_SAMPLE_BIT_COUNTER_nnout));
  DPCM_CONTROL dpcm_control_1 (
    .ACLK(ACLK), .nACLK(nACLK), .PHI1(PHI1), .D4(D4), .W4015(W4015), .nR4015(nR4015), .D7(D7), .RES(Res),
    .D6(D6), .SOUT(dpcm_sample_length_down_counter_1_sout), .R_W(R_W), .DFLOAD(dpcm_frequency_lfsr_1_dfload),
    .DOUT(dpcm_output_counter_1_dout), .nNOUT(DPCM_SAMPLE_BIT_COUNTER_nnout), .D4_2(D4_2), .DMCINT(DMCINT),
    .D7_2(D7_2), .DSSTEP(dpcm_control_1_dsstep), .DSLOAD(dpcm_control_1_dsload), .RUNDMC(RUNDMC),
    .DMCRDY(DMCRDY), .nDMC_AB(nDMC_AB), .NSTEP(dpcm_control_1_nstep), .DSTEP(dpcm_control_1_dstep),
    .PCM(dpcm_control_1_pcm), .BLOAD(dpcm_control_1_bload), .BSTEP(dpcm_control_1_bstep), .LOCK(LOCK),
    .nACLK2(nACLK2), .W4010(W4010), .DMC_EN(DMC_EN), .ENIRQ(DMC_ENIRQ), .DMC_LOOP(DMC_LOOP));
  DPCM_SAMPLE_LENGTH_DOWN_COUNTER dpcm_sample_length_down_counter_1 (
    .nACLK(nACLK), .DSLOAD(dpcm_control_1_dsload), .DSSTEP(dpcm_control_1_dsstep), .RES(Res), .LSC0(D0),
    .LSC1(D1), .LSC2(D2), .LSC3(D3), .LSC4(D4), .LSC5(D5), .LSC6(D6), .LSC7(D7),
    .SOUT(dpcm_sample_length_down_counter_1_sout), .W4013(W4013), .out_14(SAMPLE_LENGTH));
  DPCM_ADDRESS_COUNTER dpcm_address_counter_1 (
    .nACLK(nACLK), .DSLOAD(dpcm_control_1_dsload), .DSSTEP(dpcm_control_1_dsstep), .RES(Res), .LDMC6(D0),
    .LDMC7(D1), .LDMC8(D2), .LDMC9(D3), .LDMC10(D4), .LDMC11(D5), .LDMC12(D6), .LDMC13(D7), .DMC_A0(DMCA0),
    .DMC_A1(DMCA1), .DMC_A2(DMCA2), .DMC_A3(DMCA3), .DMC_A4(DMCA4), .DMC_A5(DMCA5), .DMC_A6(DMCA6),
    .DMC_A7(DMCA7), .DMC_A8(DMCA8), .DMC_A9(DMCA9), .DMC_A10(DMCA10), .DMC_A11(DMCA11), .DMC_A12(DMCA12),
    .DMC_A13(DMCA13), .DMC_A14(DMCA14), .W4012(W4012), .out_20(SAMPLE_ADR));
  Register register_1 (.D({D7, D6, D5, D4, D3, D2, D1, D0}), .clk(R_W));  // open: en, Q, clr
  DPCM_OUTPUT_COUNTER dpcm_output_counter_1 (
    .nACLK(nACLK), .W4011(W4011), .DSTEP(dpcm_control_1_dstep), .RES(Res),
    .nBOUT(dpcm_sample_shift_register_1_nbout), .D0(D0), .D1(D1), .D2(D2), .D3(D3), .D4(D4), .D5(D5),
    .D6(D6), .DMC0(DMC0), .DMC1(DMC1), .DMC2(DMC2), .DMC3(DMC3), .DMC4(DMC4), .DMC5(DMC5), .DMC6(DMC6),
    .DOUT(dpcm_output_counter_1_dout));
  DPCM_SAMPLE_SHIFT_REGISTER dpcm_sample_shift_register_1 (
    .nACLK(nACLK), .D0(D0), .D1(D1), .D2(D2), .D3(D3), .D4(D4), .D5(D5), .D6(D6), .D7(D7),
    .BSTEP(dpcm_control_1_bstep), .BLOAD(dpcm_control_1_bload), .RES(Res), .PCM(dpcm_control_1_pcm),
    .nBOUT(dpcm_sample_shift_register_1_nbout), .out_14(SAMPLE_BUF));

  // Notes on the sheet:
  //   /ACLK2 = NOT ACLK
endmodule

// FREQUENCY LFSR
module DPCM_FREQUENCY_LFSR (
  input  Res,
  input  nACLK,
  input  D0,
  input  D1,
  input  D2,
  input  D3,
  input  W4010,
  input  nACLK2,
  output [3:0] DMC_F,
  output DFLOAD
);

  wire _2_out, _5_out, and_1_out, d_ff_5_qn, d_ff_6_qn, d_ff_7_qn, d_ff_8_qn, d_ff_9_qn, d_ff_10_qn,
       d_ff_11_qn, d_ff_12_qn, d_ff_13_qn, d_ff_14_qn, d_ff_15_qn, d_ff_16_qn, d_ff_17_qn, d_ff_18_qn,
       d_ff_19_qn, d_ff_20_qn, d_ff_21_qn, d_ff_22_qn, demultiplexer_1_out0, demultiplexer_1_out1,
       demultiplexer_2_out0, demultiplexer_2_out1, demultiplexer_3_out0, demultiplexer_3_out1,
       demultiplexer_4_out0, demultiplexer_4_out1, demultiplexer_5_out0, demultiplexer_5_out1,
       demultiplexer_6_out0, demultiplexer_6_out1, demultiplexer_7_out0, demultiplexer_7_out1,
       demultiplexer_8_out0, demultiplexer_8_out1, demultiplexer_9_out0, demultiplexer_9_out1,
       demultiplexer_10_out0, demultiplexer_10_out1, dpcm_table_1_lp0, dpcm_table_1_lp1, dpcm_table_1_lp2,
       dpcm_table_1_lp3, dpcm_table_1_lp4, dpcm_table_1_lp5, dpcm_table_1_lp6, dpcm_table_1_lp7,
       dpcm_table_1_lp8, nor_1_out, nor_2_out, nor_3_out, not_1_out, not_2_out, not_3_out, not_4_out;

  not not_1 (not_1_out, nACLK);
  D_Flip_Flop #(.trigger("high")) d_ff_1 (
    .clk(not_1_out), .D(D0), .Q(DMC_F[0]), .en(W4010));  // open: Qn, preset, reset
  D_Flip_Flop #(.trigger("high")) d_ff_2 (
    .clk(not_1_out), .D(D1), .Q(DMC_F[1]), .en(W4010));  // open: Qn, preset, reset
  D_Flip_Flop #(.trigger("high")) d_ff_3 (
    .clk(not_1_out), .D(D2), .Q(DMC_F[2]), .en(W4010));  // open: Qn, preset, reset
  D_Flip_Flop #(.trigger("high")) d_ff_4 (
    .clk(not_1_out), .D(D3), .Q(DMC_F[3]), .en(W4010));  // open: Qn, preset, reset
  DPCM_TABLE dpcm_table_1 (
    .LP0(dpcm_table_1_lp0), .LP1(dpcm_table_1_lp1), .LP2(dpcm_table_1_lp2), .LP3(dpcm_table_1_lp3),
    .LP4(dpcm_table_1_lp4), .LP5(dpcm_table_1_lp5), .LP6(dpcm_table_1_lp6), .LP7(dpcm_table_1_lp7),
    .LP8(dpcm_table_1_lp8), .F3(DMC_F[3]), .F2(DMC_F[2]), .F1(DMC_F[1]), .F0(DMC_F[0]));
  not not_2 (not_2_out, nACLK2);
  nor _2 (_2_out, not_2_out, _5_out);
  not not_3 (not_3_out, _5_out);
  nor _4 (DFLOAD, not_3_out, not_2_out);
  Demultiplexer #(.enable("false")) demultiplexer_1 (
    .out0(demultiplexer_1_out0), .out1(demultiplexer_1_out1), .in(DFLOAD), .sel(dpcm_table_1_lp8));
  Demultiplexer #(.enable("false")) demultiplexer_2 (
    .out0(demultiplexer_2_out0), .out1(demultiplexer_2_out1), .in(DFLOAD), .sel(dpcm_table_1_lp7));
  Demultiplexer #(.enable("false")) demultiplexer_3 (
    .out0(demultiplexer_3_out0), .out1(demultiplexer_3_out1), .in(DFLOAD), .sel(dpcm_table_1_lp6));
  Demultiplexer #(.enable("false")) demultiplexer_4 (
    .out0(demultiplexer_4_out0), .out1(demultiplexer_4_out1), .in(DFLOAD), .sel(dpcm_table_1_lp5));
  Demultiplexer #(.enable("false")) demultiplexer_5 (
    .out0(demultiplexer_5_out0), .out1(demultiplexer_5_out1), .in(DFLOAD), .sel(dpcm_table_1_lp4));
  Demultiplexer #(.enable("false")) demultiplexer_6 (
    .out0(demultiplexer_6_out0), .out1(demultiplexer_6_out1), .in(DFLOAD), .sel(dpcm_table_1_lp3));
  Demultiplexer #(.enable("false")) demultiplexer_7 (
    .out0(demultiplexer_7_out0), .out1(demultiplexer_7_out1), .in(DFLOAD), .sel(dpcm_table_1_lp2));
  Demultiplexer #(.enable("false")) demultiplexer_8 (
    .out0(demultiplexer_8_out0), .out1(demultiplexer_8_out1), .in(DFLOAD), .sel(dpcm_table_1_lp1));
  Demultiplexer #(.enable("false")) demultiplexer_9 (
    .out0(demultiplexer_9_out0), .out1(demultiplexer_9_out1), .in(DFLOAD), .sel(dpcm_table_1_lp0));
  D_Flip_Flop #(.trigger("high")) d_ff_5 (
    .clk(_2_out), .D(nor_1_out), .Qn(d_ff_5_qn), .preset(demultiplexer_1_out1), .reset(demultiplexer_1_out0));  // open: Q, en
  D_Flip_Flop #(.trigger("high")) d_ff_6 (
    .clk(_2_out), .D(d_ff_14_qn), .Qn(d_ff_6_qn), .preset(demultiplexer_2_out1), .reset(demultiplexer_2_out0));  // open: Q, en
  D_Flip_Flop #(.trigger("high")) d_ff_7 (
    .clk(_2_out), .D(d_ff_15_qn), .Qn(d_ff_7_qn), .preset(demultiplexer_3_out1), .reset(demultiplexer_3_out0));  // open: Q, en
  D_Flip_Flop #(.trigger("high")) d_ff_8 (
    .clk(_2_out), .D(d_ff_16_qn), .Qn(d_ff_8_qn), .preset(demultiplexer_4_out1), .reset(demultiplexer_4_out0));  // open: Q, en
  D_Flip_Flop #(.trigger("high")) d_ff_9 (
    .clk(_2_out), .D(d_ff_17_qn), .Qn(d_ff_9_qn), .preset(demultiplexer_5_out1), .reset(demultiplexer_5_out0));  // open: Q, en
  D_Flip_Flop #(.trigger("high")) d_ff_10 (
    .clk(_2_out), .D(d_ff_18_qn), .Qn(d_ff_10_qn), .preset(demultiplexer_6_out1), .reset(demultiplexer_6_out0));  // open: Q, en
  D_Flip_Flop #(.trigger("high")) d_ff_11 (
    .clk(_2_out), .D(d_ff_19_qn), .Qn(d_ff_11_qn), .preset(demultiplexer_7_out1), .reset(demultiplexer_7_out0));  // open: Q, en
  D_Flip_Flop #(.trigger("high")) d_ff_12 (
    .clk(_2_out), .D(d_ff_20_qn), .Qn(d_ff_12_qn), .preset(demultiplexer_8_out1), .reset(demultiplexer_8_out0));  // open: Q, en
  D_Flip_Flop #(.trigger("high")) d_ff_13 (
    .clk(_2_out), .D(d_ff_21_qn), .Qn(d_ff_13_qn), .preset(demultiplexer_9_out1), .reset(demultiplexer_9_out0));  // open: Q, en
  nor nor_1 (nor_1_out, nor_2_out, Res, and_1_out);
  D_Flip_Flop #(.trigger("high")) d_ff_14 (.clk(nACLK), .D(d_ff_5_qn), .Qn(d_ff_14_qn));  // open: Q, preset, en, reset
  D_Flip_Flop #(.trigger("high")) d_ff_15 (.clk(nACLK), .D(d_ff_6_qn), .Qn(d_ff_15_qn));  // open: Q, preset, en, reset
  D_Flip_Flop #(.trigger("high")) d_ff_16 (.clk(nACLK), .D(d_ff_7_qn), .Qn(d_ff_16_qn));  // open: Q, preset, en, reset
  D_Flip_Flop #(.trigger("high")) d_ff_17 (.clk(nACLK), .D(d_ff_8_qn), .Qn(d_ff_17_qn));  // open: Q, preset, en, reset
  D_Flip_Flop #(.trigger("high")) d_ff_18 (.clk(nACLK), .D(d_ff_9_qn), .Qn(d_ff_18_qn));  // open: Q, preset, en, reset
  D_Flip_Flop #(.trigger("high")) d_ff_19 (.clk(nACLK), .D(d_ff_10_qn), .Qn(d_ff_19_qn));  // open: Q, preset, en, reset
  D_Flip_Flop #(.trigger("high")) d_ff_20 (.clk(nACLK), .D(d_ff_11_qn), .Qn(d_ff_20_qn));  // open: Q, preset, en, reset
  D_Flip_Flop #(.trigger("high")) d_ff_21 (.clk(nACLK), .D(d_ff_12_qn), .Qn(d_ff_21_qn));  // open: Q, preset, en, reset
  D_Flip_Flop #(.trigger("high")) d_ff_22 (.clk(nACLK), .D(d_ff_13_qn), .Qn(d_ff_22_qn));  // open: Q, preset, en, reset
  nor nor_2 (nor_2_out, d_ff_22_qn, demultiplexer_10_out0, d_ff_18_qn);
  and and_1 (and_1_out, d_ff_22_qn, d_ff_18_qn);
  nor nor_3 (nor_3_out, d_ff_14_qn, d_ff_15_qn, d_ff_16_qn, d_ff_17_qn, d_ff_18_qn, d_ff_19_qn, d_ff_20_qn, d_ff_21_qn);
  Demultiplexer #(.disabled(0), .enable("false")) demultiplexer_10 (
    .out0(demultiplexer_10_out0), .out1(demultiplexer_10_out1), .in(nor_3_out), .sel(d_ff_22_qn));
  not not_4 (not_4_out, demultiplexer_10_out1);
  nor _5 (_5_out, not_4_out, Res);

  // Notes on the sheet:
  //   1
  //   3
  //   DFSTEP
  //   S4
  //   S0
  //   6
endmodule

// DPCM TABLE
module DPCM_TABLE (
  input  F0,
  input  F1,
  input  F2,
  input  F3,
  output LP0,
  output LP1,
  output LP2,
  output LP3,
  output LP4,
  output LP5,
  output LP6,
  output LP7,
  output LP8
);

  Multiplexer #(.select(4), .width(9), .disabled(0), .enable("false")) multiplexer_1 (
    .in0(9'h173), .in1(9'h8a), .in2(9'h143), .in3(9'hdb), .in4(9'h1ee), .in5(9'h3f), .in6(9'h7d),
    .in7(9'h1d1), .in8(9'h9), .in9(9'hdc), .in10(9'hf1), .in11(9'hf9), .in12(9'h8d), .in13(9'h189),
    .in14(9'h18e), .in15(9'h156), .out({LP8, LP7, LP6, LP5, LP4, LP3, LP2, LP1, LP0}), .sel({F3, F2, F1, F0}));

  // Notes on the sheet:
  //   NTSC
  //   NTSC
  //   PAL
endmodule

module DPCM_SAMPLE_BIT_COUNTER (
  input  nACLK,
  input  NSTEP,
  input  RES,
  output nNOUT
);

  wire d_ff_1_qn, d_ff_2_qn, d_ff_3_qn, d_ff_4_qn, d_ff_5_qn, d_ff_6_qn, nor_1_out, nor_2_out, nor_3_out,
       not_1_out, not_2_out, not_3_out, xor_1_out, xor_2_out, xor_3_out;

  D_Flip_Flop #(.trigger("high")) d_ff_1 (
    .clk(NSTEP), .D(d_ff_4_qn), .Qn(d_ff_1_qn), .reset(RES));  // open: Q, preset, en
  D_Flip_Flop #(.trigger("high")) d_ff_2 (
    .clk(NSTEP), .D(d_ff_5_qn), .Qn(d_ff_2_qn), .reset(RES));  // open: Q, preset, en
  D_Flip_Flop #(.trigger("high")) d_ff_3 (
    .clk(NSTEP), .D(d_ff_6_qn), .Qn(d_ff_3_qn), .reset(RES));  // open: Q, preset, en
  xor xor_1 (xor_1_out, 1'b1, d_ff_1_qn);
  not not_1 (not_1_out, 1'b1);
  nor nor_1 (nor_1_out, not_1_out, d_ff_1_qn);
  xor xor_2 (xor_2_out, nor_1_out, d_ff_2_qn);
  not not_2 (not_2_out, nor_1_out);
  nor nor_2 (nor_2_out, not_2_out, d_ff_2_qn);
  xor xor_3 (xor_3_out, nor_2_out, d_ff_3_qn);
  not not_3 (not_3_out, nor_2_out);
  nor nor_3 (nor_3_out, not_3_out, d_ff_3_qn);
  D_Flip_Flop #(.trigger("high")) d_ff_4 (.clk(nACLK), .D(xor_1_out), .Qn(d_ff_4_qn));  // open: Q, preset, en, reset
  D_Flip_Flop #(.trigger("high")) d_ff_5 (.clk(nACLK), .D(xor_2_out), .Qn(d_ff_5_qn));  // open: Q, preset, en, reset
  D_Flip_Flop #(.trigger("high")) d_ff_6 (.clk(nACLK), .D(xor_3_out), .Qn(d_ff_6_qn));  // open: Q, preset, en, reset
  D_latch d_latch_1 (.EN(nACLK), .D(nor_3_out), .NOT_Q(nNOUT));  // open: Q
endmodule

// DPCM CONTROL
module DPCM_CONTROL (
  input  nR4015,
  input  PHI1,
  input  ACLK,
  input  nACLK,
  input  nACLK2,
  input  RES,
  input  W4015,
  input  D6,
  input  D4,
  input  D7,
  input  W4010,
  input  SOUT,
  input  DFLOAD,
  input  R_W,
  input  DOUT,
  input  LOCK,
  input  nNOUT,
  output D7_2,
  output DMCINT,
  output DMC_LOOP,
  output D4_2,
  output DMC_EN,
  output ENIRQ,
  output NSTEP,
  output DSSTEP,
  output DSLOAD,
  output RUNDMC,
  output DMCRDY,
  output nDMC_AB,
  output PCM,
  output DSTEP,
  output BLOAD,
  output BSTEP
);

  wire _3_out, _4_out, _5_out, ACLK_t, and_1_out, and_2_out, d_ff_2_qn, d_ff_3_qn, d_latch_1_q, d_latch_2_q,
       d_latch_3_not_q, d_latch_3_q, d_latch_4_not_q, d_latch_5_not_q, d_latch_6_not_q, d_latch_6_q,
       d_latch_7_not_q, d_latch_7_q, d_latch_8_q, d_latch_9_not_q, d_latch_9_q, DMASTOP, nand_1_out, nDFLOAD,
       nor_1_out, nor_2_out, nor_3_out, nor_4_out, not_3_out, not_4_out, not_5_out, not_6_out, or_1_out,
       or_2_out, PCM_DONE, s_r_ff_1_qn, s_r_ff_2_qn, s_r_ff_3_qn, s_r_ff_5_qn;

  not not_1 (ACLK_t, nACLK);
  not not_2 (nDFLOAD, DFLOAD);
  not not_3 (not_3_out, PHI1);
  nand nand_1 (nand_1_out, R_W, not_3_out);
  D_latch d_latch_1 (.EN(nACLK), .D(DOUT), .Q(d_latch_1_q));  // open: NOT_Q
  D_latch d_latch_2 (.EN(nACLK), .D(s_r_ff_5_qn), .Q(d_latch_2_q));  // open: NOT_Q
  D_Flip_Flop #(.trigger("high")) d_ff_1 (.clk(ACLK_t), .D(D6), .Q(DMC_LOOP), .en(W4010));  // open: Qn, preset, reset
  D_Flip_Flop #(.trigger("high")) d_ff_2 (
    .clk(ACLK_t), .D(D4), .Q(DMC_EN), .Qn(d_ff_2_qn), .en(W4015), .reset(or_1_out));  // open: preset
  D_Flip_Flop #(.trigger("high")) d_ff_3 (
    .clk(ACLK_t), .D(D7), .Q(ENIRQ), .Qn(d_ff_3_qn), .en(W4010));  // open: preset, reset
  nor _8 (DSTEP, nDFLOAD, d_latch_1_q, d_latch_2_q, LOCK);
  D_latch d_latch_3 (.EN(nACLK), .D(SOUT), .Q(d_latch_3_q), .NOT_Q(d_latch_3_not_q));
  D_latch d_latch_4 (.EN(nACLK), .D(DMC_EN), .NOT_Q(d_latch_4_not_q));  // open: Q
  or or_1 (or_1_out, nor_1_out, RES);
  D_latch d_latch_5 (.EN(nACLK2), .D(d_latch_4_not_q), .NOT_Q(d_latch_5_not_q));  // open: Q
  nor nor_1 (nor_1_out, d_ff_3_qn, d_latch_3_not_q, not_4_out);
  D_latch d_latch_6 (.EN(nACLK), .D(d_latch_5_not_q), .Q(d_latch_6_q), .NOT_Q(d_latch_6_not_q));
  or or_2 (or_2_out, RES, DMASTOP, d_latch_6_not_q);
  and and_1 (and_1_out, d_latch_7_q, nACLK);
  nor _3 (_3_out, ACLK, d_latch_6_q, d_latch_4_not_q);
  S_R_Flip_Flop #(.trigger("high")) s_r_ff_1 (
    .S(or_2_out), .clk(1'b1), .R(_4_out), .Qn(s_r_ff_1_qn));  // open: Q, preset, reset, en
  nor _4 (_4_out, d_latch_6_not_q, DMASTOP, nand_1_out);
  S_R_Flip_Flop #(.trigger("high")) s_r_ff_2 (
    .S(nACLK2), .clk(1'b1), .R(and_1_out), .Qn(s_r_ff_2_qn));  // open: Q, preset, reset, en
  S_R_Flip_Flop #(.trigger("high")) s_r_ff_3 (
    .S(PCM), .clk(1'b1), .R(PCM_DONE), .Qn(s_r_ff_3_qn), .reset(RES));  // open: Q, preset, en
  S_R_Flip_Flop #(.trigger("high")) s_r_ff_4 (
    .S(PCM), .clk(1'b1), .R(BLOAD), .Q(DMASTOP), .reset(RES));  // open: Qn, preset, en
  S_R_Flip_Flop #(.trigger("high")) s_r_ff_5 (
    .S(BLOAD), .clk(1'b1), .R(_5_out), .Qn(s_r_ff_5_qn), .reset(RES));  // open: Q, preset, en
  nor nor_2 (nor_2_out, nor_1_out, nor_3_out);
  nor nor_3 (nor_3_out, nor_2_out, RES, W4015, DMC_LOOP);
  not not_4 (not_4_out, PCM_DONE);
  nor _10 (PCM, nDMC_AB, PHI1);
  D_latch d_latch_7 (.EN(nACLK2), .D(s_r_ff_1_qn), .Q(d_latch_7_q), .NOT_Q(d_latch_7_not_q));
  D_latch d_latch_8 (.EN(nACLK), .D(s_r_ff_3_qn), .Q(d_latch_8_q));  // open: NOT_Q
  D_latch d_latch_9 (.EN(nACLK), .D(DMASTOP), .Q(d_latch_9_q), .NOT_Q(d_latch_9_not_q));
  nor _1 (DMCINT, nor_2_out, DMC_LOOP);
  and and_2 (and_2_out, d_latch_3_q, PCM_DONE);
  not not_5 (not_5_out, nNOUT);
  not not_6 (not_6_out, nR4015);
  assign D7_2 = not_6_out ? ~nor_2_out : 1'bz;  // Controlled_Inverter controlled_inverter_1
  assign D4_2 = not_6_out ? ~d_ff_2_qn : 1'bz;  // Controlled_Inverter controlled_inverter_2
  nor _11 (DSSTEP, not_4_out, d_latch_3_q, _3_out);
  nor nor_4 (nor_4_out, and_2_out, _3_out);
  D_latch d_latch_10 (.EN(nACLK), .D(d_latch_7_not_q), .NOT_Q(RUNDMC));  // open: Q
  nor nor_5 (DMCRDY, s_r_ff_1_qn, s_r_ff_2_qn);
  not not_7 (nDMC_AB, s_r_ff_2_qn);
  nor _8_2 (PCM_DONE, ACLK, d_latch_8_q);
  nor _5 (_5_out, nDFLOAD, d_latch_9_q, nNOUT);
  nor _9 (BLOAD, nDFLOAD, d_latch_9_not_q, nNOUT);
  nor _7 (BSTEP, nDFLOAD, not_5_out);
  not not_8 (NSTEP, nDFLOAD);
  not not_9 (DSLOAD, nor_4_out);

  // Notes on the sheet:
  //   DPCM ENABLE
  //   OUTPUT CNT OVF
  //   SAMPLE BIT CNT OVF
  //   DPCM Interrupt Control
  //   /ACLK2 = NOT ACLK
  //   DPCM Enable Control
  //   1
  //   DPCM Sample Counter Control
  //   DPCM DMA Control
  //   4
  //   DPCM Sample Buffer Control
  //   DL12
  //   DL11
  //   LENGHT = 0
  //   LOOP
  //   ED2
  //   ED2
  //   RESET ENABLE FLAG
  //   /ENIRQ
  //   DL1
  //   DL14
  //   DL3
  //   Nor2
  //   DMC2
  //   DL6
  //   ASSERT INT
  //   ED1
  //   PCM FINISH
  //   DL5
  //   CTRL2
  //   S
  //   R
  //   RS5
  //   RS6
  //   RS3
  //   RS4
  //   RS2
  //   RS1
  //   Inv10
  //   /Q
  //   Q
  //   PCM DONE
  //   DL8
  //   DL9
  //   DL10
  //   DL13
  //   LOAD SHIFT REG
  //   Delay per 1 cycle /ACLK
  //   Nor6
  //   DMC1
  //   6
  //   2
  //   DL7
  //   PCM DONE
  //   LOAD SAMPLE BUFFER
  //   STEP OUTPUT COUNTER
  //   STEP SHIFT REG
endmodule

// SAMPLE LENGTH DOWN COUNTER
module DPCM_SAMPLE_LENGTH_DOWN_COUNTER (
  input  nACLK,
  input  DSSTEP,
  input  RES,
  input  DSLOAD,
  input  W4013,
  input  LSC0,
  input  LSC1,
  input  LSC2,
  input  LSC3,
  input  LSC4,
  input  LSC5,
  input  LSC6,
  input  LSC7,
  output [7:0] out_14,
  output SOUT
);

  wire d_ff_9_q, d_ff_9_qn, d_ff_10_q, d_ff_10_qn, d_ff_11_q, d_ff_11_qn, d_ff_12_q, d_ff_12_qn, d_ff_13_q,
       d_ff_13_qn, d_ff_14_q, d_ff_14_qn, d_ff_15_q, d_ff_15_qn, d_ff_16_q, d_ff_16_qn, d_ff_17_q,
       d_ff_17_qn, d_ff_18_q, d_ff_18_qn, d_ff_19_q, d_ff_19_qn, d_ff_20_q, d_ff_20_qn, d_ff_21_qn,
       d_ff_22_qn, d_ff_23_qn, d_ff_24_qn, d_ff_25_qn, d_ff_26_qn, d_ff_27_qn, d_ff_28_qn, d_ff_29_qn,
       d_ff_30_qn, d_ff_31_qn, d_ff_32_qn, demultiplexer_1_out0, demultiplexer_1_out1, demultiplexer_2_out0,
       demultiplexer_2_out1, demultiplexer_3_out0, demultiplexer_3_out1, demultiplexer_4_out0,
       demultiplexer_4_out1, demultiplexer_5_out0, demultiplexer_5_out1, demultiplexer_6_out0,
       demultiplexer_6_out1, demultiplexer_7_out0, demultiplexer_7_out1, demultiplexer_8_out0,
       demultiplexer_8_out1, nor_1_out, nor_2_out, nor_3_out, nor_4_out, nor_5_out, nor_6_out, nor_7_out,
       nor_8_out, nor_9_out, nor_10_out, nor_11_out, not_1_out, not_2_out, not_3_out, not_4_out, not_5_out,
       not_6_out, not_7_out, not_8_out, not_9_out, not_10_out, not_11_out, not_12_out, not_13_out, or_1_out,
       or_2_out, or_3_out, or_4_out, or_5_out, or_6_out, or_7_out, or_8_out, or_9_out, xor_1_out, xor_2_out,
       xor_3_out, xor_4_out, xor_5_out, xor_6_out, xor_7_out, xor_8_out, xor_9_out, xor_10_out, xor_11_out,
       xor_12_out;

  not not_1 (not_1_out, nACLK);
  D_Flip_Flop #(.trigger("high")) d_ff_1 (
    .clk(not_1_out), .D(LSC0), .Q(out_14[0]), .en(W4013));  // open: Qn, preset, reset
  D_Flip_Flop #(.trigger("high")) d_ff_2 (
    .clk(not_1_out), .D(LSC1), .Q(out_14[1]), .en(W4013));  // open: Qn, preset, reset
  D_Flip_Flop #(.trigger("high")) d_ff_3 (
    .clk(not_1_out), .D(LSC2), .Q(out_14[2]), .en(W4013));  // open: Qn, preset, reset
  D_Flip_Flop #(.trigger("high")) d_ff_4 (
    .clk(not_1_out), .D(LSC3), .Q(out_14[3]), .en(W4013));  // open: Qn, preset, reset
  D_Flip_Flop #(.trigger("high")) d_ff_5 (
    .clk(not_1_out), .D(LSC4), .Q(out_14[4]), .en(W4013));  // open: Qn, preset, reset
  D_Flip_Flop #(.trigger("high")) d_ff_6 (
    .clk(not_1_out), .D(LSC5), .Q(out_14[5]), .en(W4013));  // open: Qn, preset, reset
  D_Flip_Flop #(.trigger("high")) d_ff_7 (
    .clk(not_1_out), .D(LSC6), .Q(out_14[6]), .en(W4013));  // open: Qn, preset, reset
  D_Flip_Flop #(.trigger("high")) d_ff_8 (
    .clk(not_1_out), .D(LSC7), .Q(out_14[7]), .en(W4013));  // open: Qn, preset, reset
  Demultiplexer #(.enable("false")) demultiplexer_1 (
    .out0(demultiplexer_1_out0), .out1(demultiplexer_1_out1), .in(DSLOAD), .sel(out_14[0]));
  Demultiplexer #(.enable("false")) demultiplexer_2 (
    .out0(demultiplexer_2_out0), .out1(demultiplexer_2_out1), .in(DSLOAD), .sel(out_14[1]));
  Demultiplexer #(.enable("false")) demultiplexer_3 (
    .out0(demultiplexer_3_out0), .out1(demultiplexer_3_out1), .in(DSLOAD), .sel(out_14[2]));
  Demultiplexer #(.enable("false")) demultiplexer_4 (
    .out0(demultiplexer_4_out0), .out1(demultiplexer_4_out1), .in(DSLOAD), .sel(out_14[3]));
  Demultiplexer #(.enable("false")) demultiplexer_5 (
    .out0(demultiplexer_5_out0), .out1(demultiplexer_5_out1), .in(DSLOAD), .sel(out_14[4]));
  Demultiplexer #(.enable("false")) demultiplexer_6 (
    .out0(demultiplexer_6_out0), .out1(demultiplexer_6_out1), .in(DSLOAD), .sel(out_14[5]));
  Demultiplexer #(.enable("false")) demultiplexer_7 (
    .out0(demultiplexer_7_out0), .out1(demultiplexer_7_out1), .in(DSLOAD), .sel(out_14[6]));
  Demultiplexer #(.enable("false")) demultiplexer_8 (
    .out0(demultiplexer_8_out0), .out1(demultiplexer_8_out1), .in(DSLOAD), .sel(out_14[7]));
  or or_1 (or_1_out, DSLOAD, RES);
  or or_2 (or_2_out, RES, demultiplexer_1_out0);
  or or_3 (or_3_out, RES, demultiplexer_2_out0);
  or or_4 (or_4_out, RES, demultiplexer_3_out0);
  or or_5 (or_5_out, RES, demultiplexer_4_out0);
  or or_6 (or_6_out, RES, demultiplexer_5_out0);
  or or_7 (or_7_out, RES, demultiplexer_6_out0);
  or or_8 (or_8_out, RES, demultiplexer_7_out0);
  or or_9 (or_9_out, RES, demultiplexer_8_out0);
  D_Flip_Flop #(.trigger("high")) d_ff_9 (
    .clk(DSSTEP), .D(d_ff_21_qn), .Q(d_ff_9_q), .Qn(d_ff_9_qn), .reset(or_1_out));  // open: preset, en
  D_Flip_Flop #(.trigger("high")) d_ff_10 (
    .clk(DSSTEP), .D(d_ff_22_qn), .Q(d_ff_10_q), .Qn(d_ff_10_qn), .reset(or_1_out));  // open: preset, en
  D_Flip_Flop #(.trigger("high")) d_ff_11 (
    .clk(DSSTEP), .D(d_ff_23_qn), .Q(d_ff_11_q), .Qn(d_ff_11_qn), .reset(or_1_out));  // open: preset, en
  D_Flip_Flop #(.trigger("high")) d_ff_12 (
    .clk(DSSTEP), .D(d_ff_24_qn), .Q(d_ff_12_q), .Qn(d_ff_12_qn), .reset(or_1_out));  // open: preset, en
  D_Flip_Flop #(.trigger("high")) d_ff_13 (
    .clk(DSSTEP), .D(d_ff_25_qn), .Q(d_ff_13_q), .Qn(d_ff_13_qn), .preset(demultiplexer_1_out1),
    .reset(or_2_out));  // open: en
  D_Flip_Flop #(.trigger("high")) d_ff_14 (
    .clk(DSSTEP), .D(d_ff_26_qn), .Q(d_ff_14_q), .Qn(d_ff_14_qn), .preset(demultiplexer_2_out1),
    .reset(or_3_out));  // open: en
  D_Flip_Flop #(.trigger("high")) d_ff_15 (
    .clk(DSSTEP), .D(d_ff_27_qn), .Q(d_ff_15_q), .Qn(d_ff_15_qn), .preset(demultiplexer_3_out1),
    .reset(or_4_out));  // open: en
  D_Flip_Flop #(.trigger("high")) d_ff_16 (
    .clk(DSSTEP), .D(d_ff_28_qn), .Q(d_ff_16_q), .Qn(d_ff_16_qn), .preset(demultiplexer_4_out1),
    .reset(or_5_out));  // open: en
  D_Flip_Flop #(.trigger("high")) d_ff_17 (
    .clk(DSSTEP), .D(d_ff_29_qn), .Q(d_ff_17_q), .Qn(d_ff_17_qn), .preset(demultiplexer_5_out1),
    .reset(or_6_out));  // open: en
  D_Flip_Flop #(.trigger("high")) d_ff_18 (
    .clk(DSSTEP), .D(d_ff_30_qn), .Q(d_ff_18_q), .Qn(d_ff_18_qn), .preset(demultiplexer_6_out1),
    .reset(or_7_out));  // open: en
  D_Flip_Flop #(.trigger("high")) d_ff_19 (
    .clk(DSSTEP), .D(d_ff_31_qn), .Q(d_ff_19_q), .Qn(d_ff_19_qn), .preset(demultiplexer_7_out1),
    .reset(or_8_out));  // open: en
  D_Flip_Flop #(.trigger("high")) d_ff_20 (
    .clk(DSSTEP), .D(d_ff_32_qn), .Q(d_ff_20_q), .Qn(d_ff_20_qn), .preset(demultiplexer_8_out1),
    .reset(or_9_out));  // open: en
  xor xor_1 (xor_1_out, 1'b1, d_ff_9_qn);
  not not_2 (not_2_out, 1'b1);
  nor nor_1 (nor_1_out, not_2_out, d_ff_9_q);
  xor xor_2 (xor_2_out, nor_1_out, d_ff_10_qn);
  not not_3 (not_3_out, nor_1_out);
  nor nor_2 (nor_2_out, not_3_out, d_ff_10_q);
  xor xor_3 (xor_3_out, nor_2_out, d_ff_11_qn);
  not not_4 (not_4_out, nor_2_out);
  nor nor_3 (nor_3_out, not_4_out, d_ff_11_q);
  xor xor_4 (xor_4_out, nor_3_out, d_ff_12_qn);
  not not_5 (not_5_out, nor_3_out);
  nor nor_4 (nor_4_out, not_5_out, d_ff_12_q);
  xor xor_5 (xor_5_out, nor_4_out, d_ff_13_qn);
  not not_6 (not_6_out, nor_4_out);
  nor nor_5 (nor_5_out, not_6_out, d_ff_13_q);
  xor xor_6 (xor_6_out, nor_5_out, d_ff_14_qn);
  not not_7 (not_7_out, nor_5_out);
  nor nor_6 (nor_6_out, not_7_out, d_ff_14_q);
  xor xor_7 (xor_7_out, nor_6_out, d_ff_15_qn);
  not not_8 (not_8_out, nor_6_out);
  nor nor_7 (nor_7_out, not_8_out, d_ff_15_q);
  xor xor_8 (xor_8_out, nor_7_out, d_ff_16_qn);
  not not_9 (not_9_out, nor_7_out);
  nor nor_8 (nor_8_out, not_9_out, d_ff_16_q);
  xor xor_9 (xor_9_out, nor_8_out, d_ff_17_qn);
  not not_10 (not_10_out, nor_8_out);
  nor nor_9 (nor_9_out, not_10_out, d_ff_17_q);
  xor xor_10 (xor_10_out, nor_9_out, d_ff_18_qn);
  not not_11 (not_11_out, nor_9_out);
  nor nor_10 (nor_10_out, not_11_out, d_ff_18_q);
  xor xor_11 (xor_11_out, nor_10_out, d_ff_19_qn);
  not not_12 (not_12_out, nor_10_out);
  nor nor_11 (nor_11_out, not_12_out, d_ff_19_q);
  xor xor_12 (xor_12_out, nor_11_out, d_ff_20_qn);
  not not_13 (not_13_out, nor_11_out);
  nor nor_12 (SOUT, not_13_out, d_ff_20_q);
  D_Flip_Flop #(.trigger("high")) d_ff_21 (.clk(nACLK), .D(xor_1_out), .Qn(d_ff_21_qn));  // open: Q, preset, en, reset
  D_Flip_Flop #(.trigger("high")) d_ff_22 (.clk(nACLK), .D(xor_2_out), .Qn(d_ff_22_qn));  // open: Q, preset, en, reset
  D_Flip_Flop #(.trigger("high")) d_ff_23 (.clk(nACLK), .D(xor_3_out), .Qn(d_ff_23_qn));  // open: Q, preset, en, reset
  D_Flip_Flop #(.trigger("high")) d_ff_24 (.clk(nACLK), .D(xor_4_out), .Qn(d_ff_24_qn));  // open: Q, preset, en, reset
  D_Flip_Flop #(.trigger("high")) d_ff_25 (.clk(nACLK), .D(xor_5_out), .Qn(d_ff_25_qn));  // open: Q, preset, en, reset
  D_Flip_Flop #(.trigger("high")) d_ff_26 (.clk(nACLK), .D(xor_6_out), .Qn(d_ff_26_qn));  // open: Q, preset, en, reset
  D_Flip_Flop #(.trigger("high")) d_ff_27 (.clk(nACLK), .D(xor_7_out), .Qn(d_ff_27_qn));  // open: Q, preset, en, reset
  D_Flip_Flop #(.trigger("high")) d_ff_28 (.clk(nACLK), .D(xor_8_out), .Qn(d_ff_28_qn));  // open: Q, preset, en, reset
  D_Flip_Flop #(.trigger("high")) d_ff_29 (.clk(nACLK), .D(xor_9_out), .Qn(d_ff_29_qn));  // open: Q, preset, en, reset
  D_Flip_Flop #(.trigger("high")) d_ff_30 (.clk(nACLK), .D(xor_10_out), .Qn(d_ff_30_qn));  // open: Q, preset, en, reset
  D_Flip_Flop #(.trigger("high")) d_ff_31 (.clk(nACLK), .D(xor_11_out), .Qn(d_ff_31_qn));  // open: Q, preset, en, reset
  D_Flip_Flop #(.trigger("high")) d_ff_32 (.clk(nACLK), .D(xor_12_out), .Qn(d_ff_32_qn));  // open: Q, preset, en, reset
endmodule

// ADDRESS COUNTER
module DPCM_ADDRESS_COUNTER (
  input  nACLK,
  input  DSSTEP,
  input  DSLOAD,
  input  RES,
  input  W4012,
  input  LDMC6,
  input  LDMC7,
  input  LDMC8,
  input  LDMC9,
  input  LDMC10,
  input  LDMC11,
  input  LDMC12,
  input  LDMC13,
  output DMC_A0,
  output DMC_A1,
  output DMC_A2,
  output DMC_A3,
  output DMC_A4,
  output DMC_A5,
  output [7:0] out_20,
  output DMC_A6,
  output DMC_A7,
  output DMC_A8,
  output DMC_A9,
  output DMC_A10,
  output DMC_A11,
  output DMC_A12,
  output DMC_A13,
  output DMC_A14
);

  wire d_ff_9_qn, d_ff_10_qn, d_ff_11_qn, d_ff_12_qn, d_ff_13_qn, d_ff_14_qn, d_ff_15_qn, d_ff_16_qn,
       d_ff_17_qn, d_ff_18_qn, d_ff_19_qn, d_ff_20_qn, d_ff_21_qn, d_ff_22_qn, d_ff_23_qn, d_ff_24_qn,
       d_ff_25_qn, d_ff_26_qn, d_ff_27_qn, d_ff_28_qn, d_ff_29_qn, d_ff_30_qn, d_ff_31_qn, d_ff_32_qn,
       d_ff_33_qn, d_ff_34_qn, d_ff_35_qn, d_ff_36_qn, d_ff_37_qn, d_ff_38_qn, demultiplexer_1_out0,
       demultiplexer_1_out1, demultiplexer_2_out0, demultiplexer_2_out1, demultiplexer_3_out0,
       demultiplexer_3_out1, demultiplexer_4_out0, demultiplexer_4_out1, demultiplexer_5_out0,
       demultiplexer_5_out1, demultiplexer_6_out0, demultiplexer_6_out1, demultiplexer_7_out0,
       demultiplexer_7_out1, demultiplexer_8_out0, demultiplexer_8_out1, nor_1_out, nor_2_out, nor_3_out,
       nor_4_out, nor_5_out, nor_6_out, nor_7_out, nor_8_out, nor_9_out, nor_10_out, nor_11_out, nor_12_out,
       nor_13_out, nor_14_out, nor_15_out, not_1_out, not_2_out, not_3_out, not_4_out, not_5_out, not_6_out,
       not_7_out, not_8_out, not_9_out, not_10_out, not_11_out, not_12_out, not_13_out, not_14_out,
       not_15_out, not_16_out, or_1_out, or_2_out, or_3_out, or_4_out, or_5_out, or_6_out, or_7_out,
       or_8_out, or_9_out, xor_1_out, xor_2_out, xor_3_out, xor_4_out, xor_5_out, xor_6_out, xor_7_out,
       xor_8_out, xor_9_out, xor_10_out, xor_11_out, xor_12_out, xor_13_out, xor_14_out, xor_15_out;

  not not_1 (not_1_out, nACLK);
  D_Flip_Flop #(.trigger("high")) d_ff_1 (
    .clk(not_1_out), .D(LDMC6), .Q(out_20[0]), .en(W4012));  // open: Qn, preset, reset
  D_Flip_Flop #(.trigger("high")) d_ff_2 (
    .clk(not_1_out), .D(LDMC7), .Q(out_20[1]), .en(W4012));  // open: Qn, preset, reset
  D_Flip_Flop #(.trigger("high")) d_ff_3 (
    .clk(not_1_out), .D(LDMC8), .Q(out_20[2]), .en(W4012));  // open: Qn, preset, reset
  D_Flip_Flop #(.trigger("high")) d_ff_4 (
    .clk(not_1_out), .D(LDMC9), .Q(out_20[3]), .en(W4012));  // open: Qn, preset, reset
  D_Flip_Flop #(.trigger("high")) d_ff_5 (
    .clk(not_1_out), .D(LDMC10), .Q(out_20[4]), .en(W4012));  // open: Qn, preset, reset
  D_Flip_Flop #(.trigger("high")) d_ff_6 (
    .clk(not_1_out), .D(LDMC11), .Q(out_20[5]), .en(W4012));  // open: Qn, preset, reset
  D_Flip_Flop #(.trigger("high")) d_ff_7 (
    .clk(not_1_out), .D(LDMC12), .Q(out_20[6]), .en(W4012));  // open: Qn, preset, reset
  D_Flip_Flop #(.trigger("high")) d_ff_8 (
    .clk(not_1_out), .D(LDMC13), .Q(out_20[7]), .en(W4012));  // open: Qn, preset, reset
  Demultiplexer #(.enable("false")) demultiplexer_1 (
    .out0(demultiplexer_1_out0), .out1(demultiplexer_1_out1), .in(DSLOAD), .sel(out_20[0]));
  Demultiplexer #(.enable("false")) demultiplexer_2 (
    .out0(demultiplexer_2_out0), .out1(demultiplexer_2_out1), .in(DSLOAD), .sel(out_20[1]));
  Demultiplexer #(.enable("false")) demultiplexer_3 (
    .out0(demultiplexer_3_out0), .out1(demultiplexer_3_out1), .in(DSLOAD), .sel(out_20[2]));
  Demultiplexer #(.enable("false")) demultiplexer_4 (
    .out0(demultiplexer_4_out0), .out1(demultiplexer_4_out1), .in(DSLOAD), .sel(out_20[3]));
  Demultiplexer #(.enable("false")) demultiplexer_5 (
    .out0(demultiplexer_5_out0), .out1(demultiplexer_5_out1), .in(DSLOAD), .sel(out_20[4]));
  Demultiplexer #(.enable("false")) demultiplexer_6 (
    .out0(demultiplexer_6_out0), .out1(demultiplexer_6_out1), .in(DSLOAD), .sel(out_20[5]));
  Demultiplexer #(.enable("false")) demultiplexer_7 (
    .out0(demultiplexer_7_out0), .out1(demultiplexer_7_out1), .in(DSLOAD), .sel(out_20[6]));
  Demultiplexer #(.enable("false")) demultiplexer_8 (
    .out0(demultiplexer_8_out0), .out1(demultiplexer_8_out1), .in(DSLOAD), .sel(out_20[7]));
  or or_1 (or_1_out, DSLOAD, RES);
  or or_2 (or_2_out, RES, demultiplexer_1_out0);
  or or_3 (or_3_out, RES, demultiplexer_2_out0);
  or or_4 (or_4_out, RES, demultiplexer_3_out0);
  or or_5 (or_5_out, RES, demultiplexer_4_out0);
  or or_6 (or_6_out, RES, demultiplexer_5_out0);
  or or_7 (or_7_out, RES, demultiplexer_6_out0);
  or or_8 (or_8_out, RES, demultiplexer_7_out0);
  or or_9 (or_9_out, RES, demultiplexer_8_out0);
  D_Flip_Flop #(.trigger("high")) d_ff_9 (
    .clk(DSSTEP), .D(d_ff_24_qn), .Q(DMC_A0), .Qn(d_ff_9_qn), .reset(or_1_out));  // open: preset, en
  D_Flip_Flop #(.trigger("high")) d_ff_10 (
    .clk(DSSTEP), .D(d_ff_25_qn), .Q(DMC_A1), .Qn(d_ff_10_qn), .reset(or_1_out));  // open: preset, en
  D_Flip_Flop #(.trigger("high")) d_ff_11 (
    .clk(DSSTEP), .D(d_ff_26_qn), .Q(DMC_A2), .Qn(d_ff_11_qn), .reset(or_1_out));  // open: preset, en
  D_Flip_Flop #(.trigger("high")) d_ff_12 (
    .clk(DSSTEP), .D(d_ff_27_qn), .Q(DMC_A3), .Qn(d_ff_12_qn), .reset(or_1_out));  // open: preset, en
  D_Flip_Flop #(.trigger("high")) d_ff_13 (
    .clk(DSSTEP), .D(d_ff_28_qn), .Q(DMC_A4), .Qn(d_ff_13_qn), .reset(or_1_out));  // open: preset, en
  D_Flip_Flop #(.trigger("high")) d_ff_14 (
    .clk(DSSTEP), .D(d_ff_29_qn), .Q(DMC_A5), .Qn(d_ff_14_qn), .reset(or_1_out));  // open: preset, en
  D_Flip_Flop #(.trigger("high")) d_ff_15 (
    .clk(DSSTEP), .D(d_ff_30_qn), .Q(DMC_A6), .Qn(d_ff_15_qn), .preset(demultiplexer_1_out1), .reset(or_2_out));  // open: en
  D_Flip_Flop #(.trigger("high")) d_ff_16 (
    .clk(DSSTEP), .D(d_ff_31_qn), .Q(DMC_A7), .Qn(d_ff_16_qn), .preset(demultiplexer_2_out1), .reset(or_3_out));  // open: en
  D_Flip_Flop #(.trigger("high")) d_ff_17 (
    .clk(DSSTEP), .D(d_ff_32_qn), .Q(DMC_A8), .Qn(d_ff_17_qn), .preset(demultiplexer_3_out1), .reset(or_4_out));  // open: en
  D_Flip_Flop #(.trigger("high")) d_ff_18 (
    .clk(DSSTEP), .D(d_ff_33_qn), .Q(DMC_A9), .Qn(d_ff_18_qn), .preset(demultiplexer_4_out1), .reset(or_5_out));  // open: en
  D_Flip_Flop #(.trigger("high")) d_ff_19 (
    .clk(DSSTEP), .D(d_ff_34_qn), .Q(DMC_A10), .Qn(d_ff_19_qn), .preset(demultiplexer_5_out1),
    .reset(or_6_out));  // open: en
  D_Flip_Flop #(.trigger("high")) d_ff_20 (
    .clk(DSSTEP), .D(d_ff_35_qn), .Q(DMC_A11), .Qn(d_ff_20_qn), .preset(demultiplexer_6_out1),
    .reset(or_7_out));  // open: en
  D_Flip_Flop #(.trigger("high")) d_ff_21 (
    .clk(DSSTEP), .D(d_ff_36_qn), .Q(DMC_A12), .Qn(d_ff_21_qn), .preset(demultiplexer_7_out1),
    .reset(or_8_out));  // open: en
  D_Flip_Flop #(.trigger("high")) d_ff_22 (
    .clk(DSSTEP), .D(d_ff_37_qn), .Q(DMC_A13), .Qn(d_ff_22_qn), .preset(demultiplexer_8_out1),
    .reset(or_9_out));  // open: en
  D_Flip_Flop #(.trigger("high")) d_ff_23 (
    .clk(DSSTEP), .D(d_ff_38_qn), .Q(DMC_A14), .Qn(d_ff_23_qn), .preset(DSLOAD), .reset(RES));  // open: en
  not not_2 (not_2_out, 1'b1);
  not not_3 (not_3_out, nor_1_out);
  not not_4 (not_4_out, nor_2_out);
  not not_5 (not_5_out, nor_3_out);
  not not_6 (not_6_out, nor_4_out);
  not not_7 (not_7_out, nor_5_out);
  not not_8 (not_8_out, nor_6_out);
  not not_9 (not_9_out, nor_7_out);
  not not_10 (not_10_out, nor_8_out);
  not not_11 (not_11_out, nor_9_out);
  not not_12 (not_12_out, nor_10_out);
  not not_13 (not_13_out, nor_11_out);
  not not_14 (not_14_out, nor_12_out);
  not not_15 (not_15_out, nor_13_out);
  not not_16 (not_16_out, nor_14_out);
  xor xor_1 (xor_1_out, 1'b1, d_ff_9_qn);
  nor nor_1 (nor_1_out, not_2_out, d_ff_9_qn);
  xor xor_2 (xor_2_out, nor_1_out, d_ff_10_qn);
  nor nor_2 (nor_2_out, not_3_out, d_ff_10_qn);
  xor xor_3 (xor_3_out, nor_2_out, d_ff_11_qn);
  nor nor_3 (nor_3_out, not_4_out, d_ff_11_qn);
  xor xor_4 (xor_4_out, nor_3_out, d_ff_12_qn);
  nor nor_4 (nor_4_out, not_5_out, d_ff_12_qn);
  xor xor_5 (xor_5_out, nor_4_out, d_ff_13_qn);
  nor nor_5 (nor_5_out, not_6_out, d_ff_13_qn);
  xor xor_6 (xor_6_out, nor_5_out, d_ff_14_qn);
  nor nor_6 (nor_6_out, not_7_out, d_ff_14_qn);
  xor xor_7 (xor_7_out, nor_6_out, d_ff_15_qn);
  nor nor_7 (nor_7_out, not_8_out, d_ff_15_qn);
  xor xor_8 (xor_8_out, nor_7_out, d_ff_16_qn);
  nor nor_8 (nor_8_out, not_9_out, d_ff_16_qn);
  xor xor_9 (xor_9_out, nor_8_out, d_ff_17_qn);
  nor nor_9 (nor_9_out, not_10_out, d_ff_17_qn);
  xor xor_10 (xor_10_out, nor_9_out, d_ff_18_qn);
  nor nor_10 (nor_10_out, not_11_out, d_ff_18_qn);
  xor xor_11 (xor_11_out, nor_10_out, d_ff_19_qn);
  nor nor_11 (nor_11_out, not_12_out, d_ff_19_qn);
  xor xor_12 (xor_12_out, nor_11_out, d_ff_20_qn);
  nor nor_12 (nor_12_out, not_13_out, d_ff_20_qn);
  xor xor_13 (xor_13_out, nor_12_out, d_ff_21_qn);
  nor nor_13 (nor_13_out, not_14_out, d_ff_21_qn);
  xor xor_14 (xor_14_out, nor_13_out, d_ff_22_qn);
  nor nor_14 (nor_14_out, not_15_out, d_ff_22_qn);
  xor xor_15 (xor_15_out, nor_14_out, d_ff_23_qn);
  nor nor_15 (nor_15_out, not_16_out, d_ff_23_qn);
  D_Flip_Flop #(.trigger("high")) d_ff_24 (.clk(nACLK), .D(xor_1_out), .Qn(d_ff_24_qn));  // open: Q, preset, en, reset
  D_Flip_Flop #(.trigger("high")) d_ff_25 (.clk(nACLK), .D(xor_2_out), .Qn(d_ff_25_qn));  // open: Q, preset, en, reset
  D_Flip_Flop #(.trigger("high")) d_ff_26 (.clk(nACLK), .D(xor_3_out), .Qn(d_ff_26_qn));  // open: Q, preset, en, reset
  D_Flip_Flop #(.trigger("high")) d_ff_27 (.clk(nACLK), .D(xor_4_out), .Qn(d_ff_27_qn));  // open: Q, preset, en, reset
  D_Flip_Flop #(.trigger("high")) d_ff_28 (.clk(nACLK), .D(xor_5_out), .Qn(d_ff_28_qn));  // open: Q, preset, en, reset
  D_Flip_Flop #(.trigger("high")) d_ff_29 (.clk(nACLK), .D(xor_6_out), .Qn(d_ff_29_qn));  // open: Q, preset, en, reset
  D_Flip_Flop #(.trigger("high")) d_ff_30 (.clk(nACLK), .D(xor_7_out), .Qn(d_ff_30_qn));  // open: Q, preset, en, reset
  D_Flip_Flop #(.trigger("high")) d_ff_31 (.clk(nACLK), .D(xor_8_out), .Qn(d_ff_31_qn));  // open: Q, preset, en, reset
  D_Flip_Flop #(.trigger("high")) d_ff_32 (.clk(nACLK), .D(xor_9_out), .Qn(d_ff_32_qn));  // open: Q, preset, en, reset
  D_Flip_Flop #(.trigger("high")) d_ff_33 (.clk(nACLK), .D(xor_10_out), .Qn(d_ff_33_qn));  // open: Q, preset, en, reset
  D_Flip_Flop #(.trigger("high")) d_ff_34 (.clk(nACLK), .D(xor_11_out), .Qn(d_ff_34_qn));  // open: Q, preset, en, reset
  D_Flip_Flop #(.trigger("high")) d_ff_35 (.clk(nACLK), .D(xor_12_out), .Qn(d_ff_35_qn));  // open: Q, preset, en, reset
  D_Flip_Flop #(.trigger("high")) d_ff_36 (.clk(nACLK), .D(xor_13_out), .Qn(d_ff_36_qn));  // open: Q, preset, en, reset
  D_Flip_Flop #(.trigger("high")) d_ff_37 (.clk(nACLK), .D(xor_14_out), .Qn(d_ff_37_qn));  // open: Q, preset, en, reset
  D_Flip_Flop #(.trigger("high")) d_ff_38 (.clk(nACLK), .D(xor_15_out), .Qn(d_ff_38_qn));  // open: Q, preset, en, reset

  // Notes on the sheet:
  //   not used
endmodule

// OUTPUT COUNTER
module DPCM_OUTPUT_COUNTER (
  input  nACLK,
  input  D0,
  input  W4011,
  input  DSTEP,
  input  nBOUT,
  input  RES,
  input  D1,
  input  D2,
  input  D3,
  input  D4,
  input  D5,
  input  D6,
  output DMC0,
  output DMC1,
  output DMC2,
  output DMC3,
  output DMC4,
  output DMC5,
  output DMC6,
  output DOUT
);

  wire d_ff_2_qn, d_ff_3_qn, d_ff_4_qn, d_ff_5_qn, d_ff_6_qn, d_ff_7_qn, d_ff_8_q, d_ff_9_q, d_ff_10_q,
       d_ff_11_q, d_ff_12_q, d_ff_13_q, demultiplexer_1_out0, demultiplexer_1_out1, demultiplexer_2_out0,
       demultiplexer_2_out1, demultiplexer_3_out0, demultiplexer_3_out1, demultiplexer_4_out0,
       demultiplexer_4_out1, demultiplexer_5_out0, demultiplexer_5_out1, demultiplexer_6_out0,
       demultiplexer_6_out1, nor_1_out, nor_2_out, nor_3_out, nor_4_out, nor_5_out, not_1_out, not_2_out,
       not_3_out, not_4_out, not_5_out, not_6_out, not_7_out, or_1_out, or_2_out, or_3_out, or_4_out,
       or_5_out, or_6_out, xor_1_out, xor_2_out, xor_3_out, xor_4_out, xor_5_out, xor_6_out, xor_7_out,
       xor_8_out, xor_9_out, xor_10_out, xor_11_out, xor_12_out;

  Demultiplexer #(.enable("false")) demultiplexer_1 (
    .out0(demultiplexer_1_out0), .out1(demultiplexer_1_out1), .in(W4011), .sel(D1));
  Demultiplexer #(.enable("false")) demultiplexer_2 (
    .out0(demultiplexer_2_out0), .out1(demultiplexer_2_out1), .in(W4011), .sel(D2));
  Demultiplexer #(.enable("false")) demultiplexer_3 (
    .out0(demultiplexer_3_out0), .out1(demultiplexer_3_out1), .in(W4011), .sel(D3));
  Demultiplexer #(.enable("false")) demultiplexer_4 (
    .out0(demultiplexer_4_out0), .out1(demultiplexer_4_out1), .in(W4011), .sel(D4));
  Demultiplexer #(.enable("false")) demultiplexer_5 (
    .out0(demultiplexer_5_out0), .out1(demultiplexer_5_out1), .in(W4011), .sel(D5));
  Demultiplexer #(.enable("false")) demultiplexer_6 (
    .out0(demultiplexer_6_out0), .out1(demultiplexer_6_out1), .in(W4011), .sel(D6));
  or or_1 (or_1_out, RES, demultiplexer_1_out0);
  or or_2 (or_2_out, RES, demultiplexer_2_out0);
  or or_3 (or_3_out, RES, demultiplexer_3_out0);
  or or_4 (or_4_out, RES, demultiplexer_4_out0);
  or or_5 (or_5_out, RES, demultiplexer_5_out0);
  or or_6 (or_6_out, RES, demultiplexer_6_out0);
  not not_1 (not_1_out, nACLK);
  D_Flip_Flop #(.trigger("high")) d_ff_1 (.clk(not_1_out), .D(D0), .Q(DMC0), .en(W4011));  // open: Qn, preset, reset
  D_Flip_Flop #(.trigger("high")) d_ff_2 (
    .clk(DSTEP), .D(d_ff_8_q), .Q(DMC1), .Qn(d_ff_2_qn), .preset(demultiplexer_1_out1), .reset(or_1_out));  // open: en
  D_Flip_Flop #(.trigger("high")) d_ff_3 (
    .clk(DSTEP), .D(d_ff_9_q), .Q(DMC2), .Qn(d_ff_3_qn), .preset(demultiplexer_2_out1), .reset(or_2_out));  // open: en
  D_Flip_Flop #(.trigger("high")) d_ff_4 (
    .clk(DSTEP), .D(d_ff_10_q), .Q(DMC3), .Qn(d_ff_4_qn), .preset(demultiplexer_3_out1), .reset(or_3_out));  // open: en
  D_Flip_Flop #(.trigger("high")) d_ff_5 (
    .clk(DSTEP), .D(d_ff_11_q), .Q(DMC4), .Qn(d_ff_5_qn), .preset(demultiplexer_4_out1), .reset(or_4_out));  // open: en
  D_Flip_Flop #(.trigger("high")) d_ff_6 (
    .clk(DSTEP), .D(d_ff_12_q), .Q(DMC5), .Qn(d_ff_6_qn), .preset(demultiplexer_5_out1), .reset(or_5_out));  // open: en
  D_Flip_Flop #(.trigger("high")) d_ff_7 (
    .clk(DSTEP), .D(d_ff_13_q), .Q(DMC6), .Qn(d_ff_7_qn), .preset(demultiplexer_6_out1), .reset(or_6_out));  // open: en
  xor xor_1 (xor_1_out, DMC1, 1'b1);
  not not_2 (not_2_out, 1'b1);
  xor xor_2 (xor_2_out, d_ff_2_qn, nBOUT);
  xor xor_3 (xor_3_out, DMC2, nor_1_out);
  not not_3 (not_3_out, nor_1_out);
  xor xor_4 (xor_4_out, d_ff_3_qn, nBOUT);
  xor xor_5 (xor_5_out, DMC3, nor_2_out);
  not not_4 (not_4_out, nor_2_out);
  xor xor_6 (xor_6_out, d_ff_4_qn, nBOUT);
  xor xor_7 (xor_7_out, DMC4, nor_3_out);
  not not_5 (not_5_out, nor_3_out);
  xor xor_8 (xor_8_out, d_ff_5_qn, nBOUT);
  xor xor_9 (xor_9_out, DMC5, nor_4_out);
  not not_6 (not_6_out, nor_4_out);
  xor xor_10 (xor_10_out, d_ff_6_qn, nBOUT);
  xor xor_11 (xor_11_out, DMC6, nor_5_out);
  not not_7 (not_7_out, nor_5_out);
  xor xor_12 (xor_12_out, d_ff_7_qn, nBOUT);
  D_Flip_Flop #(.trigger("high")) d_ff_8 (.clk(nACLK), .D(xor_1_out), .Q(d_ff_8_q));  // open: Qn, preset, en, reset
  nor nor_1 (nor_1_out, not_2_out, xor_2_out);
  D_Flip_Flop #(.trigger("high")) d_ff_9 (.clk(nACLK), .D(xor_3_out), .Q(d_ff_9_q));  // open: Qn, preset, en, reset
  nor nor_2 (nor_2_out, not_3_out, xor_4_out);
  D_Flip_Flop #(.trigger("high")) d_ff_10 (.clk(nACLK), .D(xor_5_out), .Q(d_ff_10_q));  // open: Qn, preset, en, reset
  nor nor_3 (nor_3_out, not_4_out, xor_6_out);
  D_Flip_Flop #(.trigger("high")) d_ff_11 (.clk(nACLK), .D(xor_7_out), .Q(d_ff_11_q));  // open: Qn, preset, en, reset
  nor nor_4 (nor_4_out, not_5_out, xor_8_out);
  D_Flip_Flop #(.trigger("high")) d_ff_12 (.clk(nACLK), .D(xor_9_out), .Q(d_ff_12_q));  // open: Qn, preset, en, reset
  nor nor_5 (nor_5_out, not_6_out, xor_10_out);
  D_Flip_Flop #(.trigger("high")) d_ff_13 (.clk(nACLK), .D(xor_11_out), .Q(d_ff_13_q));  // open: Qn, preset, en, reset
  nor nor_6 (DOUT, not_7_out, xor_12_out);
endmodule

// SAMPLE SHIFT REGISTER
module DPCM_SAMPLE_SHIFT_REGISTER (
  input  nACLK,
  input  BSTEP,
  input  RES,
  input  BLOAD,
  input  PCM,
  input  D0,
  input  D1,
  input  D2,
  input  D3,
  input  D4,
  input  D5,
  input  D6,
  input  D7,
  output [7:0] out_14,
  output nBOUT
);

  wire d_ff_1_qn, d_ff_2_qn, d_ff_3_qn, d_ff_4_qn, d_ff_5_qn, d_ff_6_qn, d_ff_7_qn, d_ff_8_qn, d_ff_10_qn,
       d_ff_11_qn, d_ff_12_qn, d_ff_13_qn, d_ff_14_qn, d_ff_15_qn, d_ff_16_qn, d_latch_1_not_q,
       d_latch_2_not_q, d_latch_3_not_q, d_latch_4_not_q, d_latch_5_not_q, d_latch_6_not_q, d_latch_7_not_q,
       d_latch_8_not_q, demultiplexer_1_out0, demultiplexer_1_out1, demultiplexer_2_out0,
       demultiplexer_2_out1, demultiplexer_3_out0, demultiplexer_3_out1, demultiplexer_4_out0,
       demultiplexer_4_out1, demultiplexer_5_out0, demultiplexer_5_out1, demultiplexer_6_out0,
       demultiplexer_6_out1, demultiplexer_7_out0, demultiplexer_7_out1, demultiplexer_8_out0,
       demultiplexer_8_out1, not_1_out, or_1_out, or_2_out, or_3_out, or_4_out, or_5_out, or_6_out, or_7_out,
       or_8_out;

  not not_1 (not_1_out, nACLK);
  D_Flip_Flop #(.trigger("high")) d_ff_1 (
    .clk(not_1_out), .D(D0), .Q(out_14[0]), .Qn(d_ff_1_qn), .en(PCM));  // open: preset, reset
  D_Flip_Flop #(.trigger("high")) d_ff_2 (
    .clk(not_1_out), .D(D1), .Q(out_14[1]), .Qn(d_ff_2_qn), .en(PCM));  // open: preset, reset
  D_Flip_Flop #(.trigger("high")) d_ff_3 (
    .clk(not_1_out), .D(D2), .Q(out_14[2]), .Qn(d_ff_3_qn), .en(PCM));  // open: preset, reset
  D_Flip_Flop #(.trigger("high")) d_ff_4 (
    .clk(not_1_out), .D(D3), .Q(out_14[3]), .Qn(d_ff_4_qn), .en(PCM));  // open: preset, reset
  D_Flip_Flop #(.trigger("high")) d_ff_5 (
    .clk(not_1_out), .D(D4), .Q(out_14[4]), .Qn(d_ff_5_qn), .en(PCM));  // open: preset, reset
  D_Flip_Flop #(.trigger("high")) d_ff_6 (
    .clk(not_1_out), .D(D5), .Q(out_14[5]), .Qn(d_ff_6_qn), .en(PCM));  // open: preset, reset
  D_Flip_Flop #(.trigger("high")) d_ff_7 (
    .clk(not_1_out), .D(D6), .Q(out_14[6]), .Qn(d_ff_7_qn), .en(PCM));  // open: preset, reset
  D_Flip_Flop #(.trigger("high")) d_ff_8 (
    .clk(not_1_out), .D(D7), .Q(out_14[7]), .Qn(d_ff_8_qn), .en(PCM));  // open: preset, reset
  Demultiplexer #(.enable("false")) demultiplexer_1 (
    .out0(demultiplexer_1_out0), .out1(demultiplexer_1_out1), .in(BLOAD), .sel(d_ff_1_qn));
  Demultiplexer #(.enable("false")) demultiplexer_2 (
    .out0(demultiplexer_2_out0), .out1(demultiplexer_2_out1), .in(BLOAD), .sel(d_ff_2_qn));
  Demultiplexer #(.enable("false")) demultiplexer_3 (
    .out0(demultiplexer_3_out0), .out1(demultiplexer_3_out1), .in(BLOAD), .sel(d_ff_3_qn));
  Demultiplexer #(.enable("false")) demultiplexer_4 (
    .out0(demultiplexer_4_out0), .out1(demultiplexer_4_out1), .in(BLOAD), .sel(d_ff_4_qn));
  Demultiplexer #(.enable("false")) demultiplexer_5 (
    .out0(demultiplexer_5_out0), .out1(demultiplexer_5_out1), .in(BLOAD), .sel(d_ff_5_qn));
  Demultiplexer #(.enable("false")) demultiplexer_6 (
    .out0(demultiplexer_6_out0), .out1(demultiplexer_6_out1), .in(BLOAD), .sel(d_ff_6_qn));
  Demultiplexer #(.enable("false")) demultiplexer_7 (
    .out0(demultiplexer_7_out0), .out1(demultiplexer_7_out1), .in(BLOAD), .sel(d_ff_7_qn));
  Demultiplexer #(.enable("false")) demultiplexer_8 (
    .out0(demultiplexer_8_out0), .out1(demultiplexer_8_out1), .in(BLOAD), .sel(d_ff_8_qn));
  or or_1 (or_1_out, demultiplexer_1_out1, RES);
  or or_2 (or_2_out, demultiplexer_2_out1, RES);
  or or_3 (or_3_out, demultiplexer_3_out1, RES);
  or or_4 (or_4_out, demultiplexer_4_out1, RES);
  or or_5 (or_5_out, demultiplexer_5_out1, RES);
  or or_6 (or_6_out, demultiplexer_6_out1, RES);
  or or_7 (or_7_out, demultiplexer_7_out1, RES);
  or or_8 (or_8_out, demultiplexer_8_out1, RES);
  D_latch d_latch_1 (.EN(nACLK), .D(d_ff_10_qn), .NOT_Q(d_latch_1_not_q));  // open: Q
  D_latch d_latch_2 (.EN(nACLK), .D(d_ff_11_qn), .NOT_Q(d_latch_2_not_q));  // open: Q
  D_latch d_latch_3 (.EN(nACLK), .D(d_ff_12_qn), .NOT_Q(d_latch_3_not_q));  // open: Q
  D_latch d_latch_4 (.EN(nACLK), .D(d_ff_13_qn), .NOT_Q(d_latch_4_not_q));  // open: Q
  D_latch d_latch_5 (.EN(nACLK), .D(d_ff_14_qn), .NOT_Q(d_latch_5_not_q));  // open: Q
  D_latch d_latch_6 (.EN(nACLK), .D(d_ff_15_qn), .NOT_Q(d_latch_6_not_q));  // open: Q
  D_latch d_latch_7 (.EN(nACLK), .D(d_ff_16_qn), .NOT_Q(d_latch_7_not_q));  // open: Q
  D_latch d_latch_8 (.EN(nACLK), .D(1'b0), .NOT_Q(d_latch_8_not_q));  // open: Q
  D_Flip_Flop #(.trigger("high")) d_ff_9 (
    .clk(BSTEP), .D(d_latch_1_not_q), .Q(nBOUT), .preset(or_1_out), .reset(demultiplexer_1_out0));  // open: Qn, en
  D_Flip_Flop #(.trigger("high")) d_ff_10 (
    .clk(BSTEP), .D(d_latch_2_not_q), .Qn(d_ff_10_qn), .preset(or_2_out), .reset(demultiplexer_2_out0));  // open: Q, en
  D_Flip_Flop #(.trigger("high")) d_ff_11 (
    .clk(BSTEP), .D(d_latch_3_not_q), .Qn(d_ff_11_qn), .preset(or_3_out), .reset(demultiplexer_3_out0));  // open: Q, en
  D_Flip_Flop #(.trigger("high")) d_ff_12 (
    .clk(BSTEP), .D(d_latch_4_not_q), .Qn(d_ff_12_qn), .preset(or_4_out), .reset(demultiplexer_4_out0));  // open: Q, en
  D_Flip_Flop #(.trigger("high")) d_ff_13 (
    .clk(BSTEP), .D(d_latch_5_not_q), .Qn(d_ff_13_qn), .preset(or_5_out), .reset(demultiplexer_5_out0));  // open: Q, en
  D_Flip_Flop #(.trigger("high")) d_ff_14 (
    .clk(BSTEP), .D(d_latch_6_not_q), .Qn(d_ff_14_qn), .preset(or_6_out), .reset(demultiplexer_6_out0));  // open: Q, en
  D_Flip_Flop #(.trigger("high")) d_ff_15 (
    .clk(BSTEP), .D(d_latch_7_not_q), .Qn(d_ff_15_qn), .preset(or_7_out), .reset(demultiplexer_7_out0));  // open: Q, en
  D_Flip_Flop #(.trigger("high")) d_ff_16 (
    .clk(BSTEP), .D(d_latch_8_not_q), .Qn(d_ff_16_qn), .preset(or_8_out), .reset(demultiplexer_8_out0));  // open: Q, en

  // Notes on the sheet:
  //   SAMPLE REGISTER
endmodule

// SPRITE DMA
module SPRITE_DMA (
  input  ACLK,
  input  nACLK,
  input  PHI1,
  input  PHI2,
  input  nR4015,
  input  nDBGRD,
  input  R_W__CPU,
  input  D0,
  input  D1,
  input  D2,
  input  D3,
  input  D4,
  input  D5,
  input  D6,
  input  D7,
  input  W4014,
  input  RES,
  input  D0_2,
  input  D1_2,
  input  D2_2,
  input  RUNDMC,
  input  D3_2,
  input  DMC_RDY,
  input  D4_2,
  input  D5_2,
  input  D6_2,
  input  nDMC_AB,
  input  D7_2,
  input  CPUA0,
  input  CPUA1,
  input  CPUA2,
  input  CPUA3,
  input  CPUA4,
  input  CPUA5,
  input  CPUA6,
  input  CPUA7,
  input  CPUA8,
  input  CPUA9,
  input  CPUA10,
  input  CPUA11,
  input  CPUA12,
  input  CPUA13,
  input  CPUA14,
  input  CPUA15,
  input  DMC0,
  input  DMC1,
  input  DMC2,
  input  DMC3,
  input  DMC4,
  input  DMC5,
  input  DMC6,
  input  DMC7,
  input  DMC8,
  input  DMC9,
  input  DMC10,
  input  DMC11,
  input  DMC12,
  input  DMC13,
  input  DMC14,
  output D0_3,
  output D1_3,
  output D2_3,
  output D3_3,
  output D4_3,
  output D5_3,
  output D6_3,
  output D7_3,
  output WR,
  output R_W__to_R_W_ic_pin,
  output RDY,
  output SPR_PPU,
  output A0,
  output A1,
  output A2,
  output A3,
  output A4,
  output A5,
  output A6,
  output A7,
  output A8,
  output A9,
  output A10,
  output A11,
  output A12,
  output A13,
  output A14,
  output A15
);

  wire d_ff_1_qn, d_ff_2_qn, d_ff_3_qn, d_ff_4_qn, d_ff_5_qn, d_ff_6_qn, d_ff_7_qn, d_ff_8_qn,
       dma_address_counter_1_spre, dma_control_1_sprs, nor_2_out, not_1_out, not_2_out, not_3_out, SPR_CPU;
  wire [15:0] dma_address_counter_1_spra0;

  not not_1 (not_1_out, R_W__CPU);
  not not_2 (not_2_out, ACLK);
  nor nor_1 (R_W__to_R_W_ic_pin, SPR_PPU, not_1_out);
  DMA_ADDRESS_COUNTER dma_address_counter_1 (
    .nACLK(nACLK), .SPRS(dma_control_1_sprs), .W4014(W4014), .RES(RES), .D0(D0), .D1(D1), .D2(D2), .D3(D3),
    .D4(D4), .D5(D5), .D6(D6), .D7(D7), .SPRA0(dma_address_counter_1_spra0[0]),
    .SPRA1(dma_address_counter_1_spra0[1]), .SPRA2(dma_address_counter_1_spra0[2]),
    .SPRA3(dma_address_counter_1_spra0[3]), .SPRA4(dma_address_counter_1_spra0[4]),
    .SPRA5(dma_address_counter_1_spra0[5]), .SPRA6(dma_address_counter_1_spra0[6]),
    .SPRA7(dma_address_counter_1_spra0[7]), .SPRA8(dma_address_counter_1_spra0[8]),
    .SPRA9(dma_address_counter_1_spra0[9]), .SPRA10(dma_address_counter_1_spra0[10]),
    .SPRA11(dma_address_counter_1_spra0[11]), .SPRA12(dma_address_counter_1_spra0[12]),
    .SPRA13(dma_address_counter_1_spra0[13]), .SPRA14(dma_address_counter_1_spra0[14]),
    .SPRA15(dma_address_counter_1_spra0[15]), .SPRE(dma_address_counter_1_spre));
  DMA_CONTROL dma_control_1 (
    .nACLK2(not_2_out), .PHI1(PHI1), .nACLK(nACLK), .W4014(W4014), .SPRE(dma_address_counter_1_spre),
    .RUNDMC(RUNDMC), .DMCRDY(DMC_RDY), .R_W(R_W__CPU), .RES(RES), .SPRS(dma_control_1_sprs), .RDY(RDY),
    .SPR_PPU(SPR_PPU), .SPR_CPU(SPR_CPU));
  nand nand_1 (WR, nR4015, nDBGRD, R_W__to_R_W_ic_pin);
  not not_3 (not_3_out, nDMC_AB);
  nor nor_2 (nor_2_out, SPR_CPU, SPR_PPU, not_3_out);
  assign {A15, A14, A13, A12, A11, A10, A9, A8, A7, A6, A5, A4, A3, A2, A1, A0} = SPR_CPU ? dma_address_counter_1_spra0 : 16'bz;  // Controlled_Buffer controlled_buffer_1
  assign {A15, A14, A13, A12, A11, A10, A9, A8, A7, A6, A5, A4, A3, A2, A1, A0} = nor_2_out ? {CPUA15, CPUA14, CPUA13, CPUA12, CPUA11, CPUA10, CPUA9, CPUA8, CPUA7, CPUA6, CPUA5, CPUA4, CPUA3, CPUA2, CPUA1, CPUA0} : 16'bz;  // Controlled_Buffer controlled_buffer_2
  assign {A15, A14, A13, A12, A11, A10, A9, A8, A7, A6, A5, A4, A3, A2, A1, A0} = SPR_PPU ? 16'h2004 : 16'bz;  // Controlled_Buffer controlled_buffer_3
  assign {A15, A14, A13, A12, A11, A10, A9, A8, A7, A6, A5, A4, A3, A2, A1, A0} = not_3_out ? {1'b1, DMC14, DMC13, DMC12, DMC11, DMC10, DMC9, DMC8, DMC7, DMC6, DMC5, DMC4, DMC3, DMC2, DMC1, DMC0} : 16'bz;  // Controlled_Buffer controlled_buffer_4
  D_Flip_Flop #(.trigger("high")) d_ff_1 (
    .clk(PHI2), .D(D0_2), .Qn(d_ff_1_qn), .en(SPR_CPU));  // open: Q, preset, reset
  D_Flip_Flop #(.trigger("high")) d_ff_2 (
    .clk(PHI2), .D(D1_2), .Qn(d_ff_2_qn), .en(SPR_CPU));  // open: Q, preset, reset
  D_Flip_Flop #(.trigger("high")) d_ff_3 (
    .clk(PHI2), .D(D2_2), .Qn(d_ff_3_qn), .en(SPR_CPU));  // open: Q, preset, reset
  D_Flip_Flop #(.trigger("high")) d_ff_4 (
    .clk(PHI2), .D(D3_2), .Qn(d_ff_4_qn), .en(SPR_CPU));  // open: Q, preset, reset
  D_Flip_Flop #(.trigger("high")) d_ff_5 (
    .clk(PHI2), .D(D4_2), .Qn(d_ff_5_qn), .en(SPR_CPU));  // open: Q, preset, reset
  D_Flip_Flop #(.trigger("high")) d_ff_6 (
    .clk(PHI2), .D(D5_2), .Qn(d_ff_6_qn), .en(SPR_CPU));  // open: Q, preset, reset
  D_Flip_Flop #(.trigger("high")) d_ff_7 (
    .clk(PHI2), .D(D6_2), .Qn(d_ff_7_qn), .en(SPR_CPU));  // open: Q, preset, reset
  D_Flip_Flop #(.trigger("high")) d_ff_8 (
    .clk(PHI2), .D(D7_2), .Qn(d_ff_8_qn), .en(SPR_CPU));  // open: Q, preset, reset
  assign D0_3 = SPR_PPU ? ~d_ff_1_qn : 1'bz;  // Controlled_Inverter controlled_inverter_1
  assign D1_3 = SPR_PPU ? ~d_ff_2_qn : 1'bz;  // Controlled_Inverter controlled_inverter_2
  assign D2_3 = SPR_PPU ? ~d_ff_3_qn : 1'bz;  // Controlled_Inverter controlled_inverter_3
  assign D3_3 = SPR_PPU ? ~d_ff_4_qn : 1'bz;  // Controlled_Inverter controlled_inverter_4
  assign D4_3 = SPR_PPU ? ~d_ff_5_qn : 1'bz;  // Controlled_Inverter controlled_inverter_5
  assign D5_3 = SPR_PPU ? ~d_ff_6_qn : 1'bz;  // Controlled_Inverter controlled_inverter_6
  assign D6_3 = SPR_PPU ? ~d_ff_7_qn : 1'bz;  // Controlled_Inverter controlled_inverter_7
  assign D7_3 = SPR_PPU ? ~d_ff_8_qn : 1'bz;  // Controlled_Inverter controlled_inverter_8

  // Notes on the sheet:
  //   INV1
  //   NOR1
  //   ADDRESS  MUX
  //   0010000000000100
  //   $2004
  //   If /R4015 (read 4015) then disable data buffer (2a03 databus become Z)
  //   SPRITE DMA BUFFER
endmodule

// DMA ADDRESS COUNTER
module DMA_ADDRESS_COUNTER (
  input  nACLK,
  input  SPRS,
  input  RES,
  input  W4014,
  input  D0,
  input  D1,
  input  D2,
  input  D3,
  input  D4,
  input  D5,
  input  D6,
  input  D7,
  output SPRA0,
  output SPRA1,
  output SPRA2,
  output SPRA3,
  output SPRA4,
  output SPRA5,
  output SPRA6,
  output SPRA7,
  output SPRA8,
  output SPRA9,
  output SPRA10,
  output SPRA11,
  output SPRA12,
  output SPRA13,
  output SPRA14,
  output SPRA15,
  output SPRE
);

  wire d_ff_9_qn, d_ff_10_qn, d_ff_11_qn, d_ff_12_qn, d_ff_13_qn, d_ff_14_qn, d_ff_15_qn, d_ff_16_qn,
       d_ff_17_qn, d_ff_18_qn, d_ff_19_qn, d_ff_20_qn, d_ff_21_qn, d_ff_22_qn, d_ff_23_qn, d_ff_24_qn,
       nor_1_out, nor_2_out, nor_3_out, nor_4_out, nor_5_out, nor_6_out, nor_7_out, not_1_out, not_2_out,
       not_3_out, not_4_out, not_5_out, not_6_out, not_7_out, not_8_out, not_9_out, or_1_out, xor_1_out,
       xor_2_out, xor_3_out, xor_4_out, xor_5_out, xor_6_out, xor_7_out, xor_8_out;

  not not_1 (not_1_out, nACLK);
  or or_1 (or_1_out, RES, W4014);
  D_Flip_Flop #(.trigger("high")) d_ff_1 (.clk(not_1_out), .D(D0), .Q(SPRA8), .en(W4014));  // open: Qn, preset, reset
  D_Flip_Flop #(.trigger("high")) d_ff_2 (.clk(not_1_out), .D(D1), .Q(SPRA9), .en(W4014));  // open: Qn, preset, reset
  D_Flip_Flop #(.trigger("high")) d_ff_3 (.clk(not_1_out), .D(D2), .Q(SPRA10), .en(W4014));  // open: Qn, preset, reset
  D_Flip_Flop #(.trigger("high")) d_ff_4 (.clk(not_1_out), .D(D3), .Q(SPRA11), .en(W4014));  // open: Qn, preset, reset
  D_Flip_Flop #(.trigger("high")) d_ff_5 (.clk(not_1_out), .D(D4), .Q(SPRA12), .en(W4014));  // open: Qn, preset, reset
  D_Flip_Flop #(.trigger("high")) d_ff_6 (.clk(not_1_out), .D(D5), .Q(SPRA13), .en(W4014));  // open: Qn, preset, reset
  D_Flip_Flop #(.trigger("high")) d_ff_7 (.clk(not_1_out), .D(D6), .Q(SPRA14), .en(W4014));  // open: Qn, preset, reset
  D_Flip_Flop #(.trigger("high")) d_ff_8 (.clk(not_1_out), .D(D7), .Q(SPRA15), .en(W4014));  // open: Qn, preset, reset
  D_Flip_Flop #(.trigger("high")) d_ff_9 (
    .clk(SPRS), .D(d_ff_17_qn), .Q(SPRA0), .Qn(d_ff_9_qn), .reset(or_1_out));  // open: preset, en
  D_Flip_Flop #(.trigger("high")) d_ff_10 (
    .clk(SPRS), .D(d_ff_18_qn), .Q(SPRA1), .Qn(d_ff_10_qn), .reset(or_1_out));  // open: preset, en
  D_Flip_Flop #(.trigger("high")) d_ff_11 (
    .clk(SPRS), .D(d_ff_19_qn), .Q(SPRA2), .Qn(d_ff_11_qn), .reset(or_1_out));  // open: preset, en
  D_Flip_Flop #(.trigger("high")) d_ff_12 (
    .clk(SPRS), .D(d_ff_20_qn), .Q(SPRA3), .Qn(d_ff_12_qn), .reset(or_1_out));  // open: preset, en
  D_Flip_Flop #(.trigger("high")) d_ff_13 (
    .clk(SPRS), .D(d_ff_21_qn), .Q(SPRA4), .Qn(d_ff_13_qn), .reset(or_1_out));  // open: preset, en
  D_Flip_Flop #(.trigger("high")) d_ff_14 (
    .clk(SPRS), .D(d_ff_22_qn), .Q(SPRA5), .Qn(d_ff_14_qn), .reset(or_1_out));  // open: preset, en
  D_Flip_Flop #(.trigger("high")) d_ff_15 (
    .clk(SPRS), .D(d_ff_23_qn), .Q(SPRA6), .Qn(d_ff_15_qn), .reset(or_1_out));  // open: preset, en
  D_Flip_Flop #(.trigger("high")) d_ff_16 (
    .clk(SPRS), .D(d_ff_24_qn), .Q(SPRA7), .Qn(d_ff_16_qn), .reset(or_1_out));  // open: preset, en
  not not_2 (not_2_out, 1'b1);
  not not_3 (not_3_out, nor_1_out);
  not not_4 (not_4_out, nor_2_out);
  not not_5 (not_5_out, nor_3_out);
  not not_6 (not_6_out, nor_4_out);
  not not_7 (not_7_out, nor_5_out);
  not not_8 (not_8_out, nor_6_out);
  not not_9 (not_9_out, nor_7_out);
  xor xor_1 (xor_1_out, 1'b1, d_ff_9_qn);
  nor nor_1 (nor_1_out, d_ff_9_qn, not_2_out);
  xor xor_2 (xor_2_out, nor_1_out, d_ff_10_qn);
  nor nor_2 (nor_2_out, d_ff_10_qn, not_3_out);
  xor xor_3 (xor_3_out, nor_2_out, d_ff_11_qn);
  nor nor_3 (nor_3_out, d_ff_11_qn, not_4_out);
  xor xor_4 (xor_4_out, nor_3_out, d_ff_12_qn);
  nor nor_4 (nor_4_out, d_ff_12_qn, not_5_out);
  xor xor_5 (xor_5_out, nor_4_out, d_ff_13_qn);
  nor nor_5 (nor_5_out, d_ff_13_qn, not_6_out);
  xor xor_6 (xor_6_out, nor_5_out, d_ff_14_qn);
  nor nor_6 (nor_6_out, d_ff_14_qn, not_7_out);
  xor xor_7 (xor_7_out, nor_6_out, d_ff_15_qn);
  nor nor_7 (nor_7_out, d_ff_15_qn, not_8_out);
  xor xor_8 (xor_8_out, nor_7_out, d_ff_16_qn);
  nor nor_8 (SPRE, d_ff_16_qn, not_9_out);
  D_Flip_Flop #(.trigger("high")) d_ff_17 (.clk(nACLK), .D(xor_1_out), .Qn(d_ff_17_qn));  // open: Q, preset, en, reset
  D_Flip_Flop #(.trigger("high")) d_ff_18 (.clk(nACLK), .D(xor_2_out), .Qn(d_ff_18_qn));  // open: Q, preset, en, reset
  D_Flip_Flop #(.trigger("high")) d_ff_19 (.clk(nACLK), .D(xor_3_out), .Qn(d_ff_19_qn));  // open: Q, preset, en, reset
  D_Flip_Flop #(.trigger("high")) d_ff_20 (.clk(nACLK), .D(xor_4_out), .Qn(d_ff_20_qn));  // open: Q, preset, en, reset
  D_Flip_Flop #(.trigger("high")) d_ff_21 (.clk(nACLK), .D(xor_5_out), .Qn(d_ff_21_qn));  // open: Q, preset, en, reset
  D_Flip_Flop #(.trigger("high")) d_ff_22 (.clk(nACLK), .D(xor_6_out), .Qn(d_ff_22_qn));  // open: Q, preset, en, reset
  D_Flip_Flop #(.trigger("high")) d_ff_23 (.clk(nACLK), .D(xor_7_out), .Qn(d_ff_23_qn));  // open: Q, preset, en, reset
  D_Flip_Flop #(.trigger("high")) d_ff_24 (.clk(nACLK), .D(xor_8_out), .Qn(d_ff_24_qn));  // open: Q, preset, en, reset
endmodule

// DMA CONTROL
module DMA_CONTROL (
  input  nACLK2,
  input  nACLK,
  input  RUNDMC,
  input  SPRE,
  input  RES,
  input  W4014,
  input  PHI1,
  input  R_W,
  input  DMCRDY,
  output SPR_PPU,
  output SPR_CPU,
  output SPRS,
  output RDY
);

  wire _1_2_out, _1_out, _2_out, _7_out, _8_out, _9_out, _10_out, _13_out, _14_out, _15_out, _16_out,
       d_latch_1_q, d_latch_2_not_q, d_latch_2_q, d_latch_3_q, not_1_out, not_2_out;

  nor _15 (_15_out, nACLK2, _16_out);
  nor _16 (_16_out, _15_out, nACLK);
  not not_1 (not_1_out, PHI1);
  not not_2 (not_2_out, nACLK2);
  D_latch d_latch_1 (.EN(nACLK), .D(SPRE), .Q(d_latch_1_q));  // open: NOT_Q
  D_latch d_latch_2 (.EN(nACLK), .D(_1_2_out), .Q(d_latch_2_q), .NOT_Q(d_latch_2_not_q));
  nor _8 (_8_out, d_latch_2_q, RES, _7_out);
  nor _7 (_7_out, _8_out, W4014);
  D_latch d_latch_3 (.EN(nACLK2), .D(_7_out), .Q(d_latch_3_q));  // open: NOT_Q
  nand _13 (_13_out, not_1_out, R_W);
  nor _17 (SPR_PPU, _15_out, RUNDMC, d_latch_2_not_q);
  nor _18 (SPR_CPU, RUNDMC, d_latch_2_not_q, _16_out);
  nor _3 (SPRS, RUNDMC, d_latch_2_not_q, not_2_out);
  nor _9 (_9_out, d_latch_2_q, _8_out);
  nor _14 (_14_out, d_latch_3_q, _13_out);
  and _1 (_1_out, SPRS, d_latch_1_q);
  nand _10 (_10_out, _9_out, DMCRDY);
  nor _1_2 (_1_2_out, _1_out, RES, _2_out);
  nor _2 (_2_out, _1_2_out, _14_out);
  not not_3 (RDY, _10_out);

  // Notes on the sheet:
  //   RS3
  //   DMA DIR TOGGLE
  //   1
  //   5
  //   R
  //   RS1
  //   START  DMA
  //   S
  //   14
  //   12
  //   NO Spr
  //   Q
  //   /Q
  //   INCREMENT  DMA ADR
  //   S
  //   RS2
  //   STOP  DMA
  //   R
  //   DO Spr
  //   /Q
  //   Q
  //   11
endmodule
// LENGTH TABLE
module LENGTH_TABLE (
  input  D3,
  input  D4,
  input  D5,
  input  D6,
  input  D7,
  output LC0,
  output LC1,
  output LC2,
  output LC3,
  output LC4,
  output LC5,
  output LC6,
  output LC7
);

  Multiplexer #(.select(5), .width(8), .disabled(0), .enable("false")) multiplexer_1 (
    .in0(8'h9), .in1(8'hfd), .in2(8'h13), .in3(8'h1), .in4(8'h27), .in5(8'h3), .in6(8'h4f), .in7(8'h5),
    .in8(8'h9f), .in9(8'h7), .in10(8'h3b), .in11(8'h9), .in12(8'hd), .in13(8'hb), .in14(8'h19), .in15(8'hd),
    .in16(8'hb), .in17(8'hf), .in18(8'h17), .in19(8'h11), .in20(8'h2f), .in21(8'h13), .in22(8'h5f),
    .in23(8'h15), .in24(8'hbf), .in25(8'h17), .in26(8'h47), .in27(8'h19), .in28(8'hf), .in29(8'h1b),
    .in30(8'h1f), .in31(8'h1d), .out({LC7, LC6, LC5, LC4, LC3, LC2, LC1, LC0}), .sel({D7, D6, D5, D4, D3}));
  D_latch d_latch_1 (.EN(1'b1));  // open: D, Q, NOT_Q
  D_latch d_latch_2 (.EN(1'b1));  // open: D, Q, NOT_Q
  D_latch d_latch_3 (.EN(1'b1));  // open: D, Q, NOT_Q
  D_latch d_latch_4 (.EN(1'b1));  // open: D, Q, NOT_Q
  D_latch d_latch_5 (.EN(1'b1));  // open: D, Q, NOT_Q

  // Notes on the sheet:
  //   NTSC = PAL
endmodule

// LENGTH DOWN COUNTER
module LENGTH_DOWN_COUNTER (
  input  nACLK,
  input  nACLK4,
  input  W4015,
  input  Dx,
  input  nLFO2,
  input  nR4015,
  input  W400x,
  input  RES,
  input  HALT,
  input  LC0,
  input  LC1,
  input  LC2,
  input  LC3,
  input  LC4,
  input  LC5,
  input  LC6,
  input  LC7,
  output NOxxx,
  output Dx_2
);

  wire d_ff_1_q, d_ff_1_qn, d_ff_2_q, d_ff_2_qn, d_ff_3_q, d_ff_3_qn, d_ff_4_q, d_ff_4_qn, d_ff_5_q,
       d_ff_5_qn, d_ff_6_q, d_ff_6_qn, d_ff_7_q, d_ff_7_qn, d_ff_8_q, d_ff_8_qn, d_ff_9_qn, d_ff_10_qn,
       d_ff_11_qn, d_ff_12_qn, d_ff_13_qn, d_ff_14_qn, d_ff_15_qn, d_ff_16_qn, demultiplexer_1_out0,
       demultiplexer_1_out1, demultiplexer_2_out0, demultiplexer_2_out1, demultiplexer_3_out0,
       demultiplexer_3_out1, demultiplexer_4_out0, demultiplexer_4_out1, demultiplexer_5_out0,
       demultiplexer_5_out1, demultiplexer_6_out0, demultiplexer_6_out1, demultiplexer_7_out0,
       demultiplexer_7_out1, demultiplexer_8_out0, demultiplexer_8_out1, length_control_1_step, nor_1_out,
       nor_2_out, nor_3_out, nor_4_out, nor_5_out, nor_6_out, nor_7_out, nor_8_out, not_1_out, not_2_out,
       not_3_out, not_4_out, not_5_out, not_6_out, not_7_out, not_8_out, or_1_out, or_2_out, or_3_out,
       or_4_out, or_5_out, or_6_out, or_7_out, or_8_out, xor_1_out, xor_2_out, xor_3_out, xor_4_out,
       xor_5_out, xor_6_out, xor_7_out, xor_8_out;

  Demultiplexer #(.enable("false")) demultiplexer_1 (
    .out0(demultiplexer_1_out0), .out1(demultiplexer_1_out1), .in(W400x), .sel(LC0));
  Demultiplexer #(.enable("false")) demultiplexer_2 (
    .out0(demultiplexer_2_out0), .out1(demultiplexer_2_out1), .in(W400x), .sel(LC1));
  Demultiplexer #(.enable("false")) demultiplexer_3 (
    .out0(demultiplexer_3_out0), .out1(demultiplexer_3_out1), .in(W400x), .sel(LC2));
  Demultiplexer #(.enable("false")) demultiplexer_4 (
    .out0(demultiplexer_4_out0), .out1(demultiplexer_4_out1), .in(W400x), .sel(LC3));
  Demultiplexer #(.enable("false")) demultiplexer_5 (
    .out0(demultiplexer_5_out0), .out1(demultiplexer_5_out1), .in(W400x), .sel(LC4));
  Demultiplexer #(.enable("false")) demultiplexer_6 (
    .out0(demultiplexer_6_out0), .out1(demultiplexer_6_out1), .in(W400x), .sel(LC5));
  Demultiplexer #(.enable("false")) demultiplexer_7 (
    .out0(demultiplexer_7_out0), .out1(demultiplexer_7_out1), .in(W400x), .sel(LC6));
  Demultiplexer #(.enable("false")) demultiplexer_8 (
    .out0(demultiplexer_8_out0), .out1(demultiplexer_8_out1), .in(W400x), .sel(LC7));
  or or_1 (or_1_out, RES, demultiplexer_1_out0);
  or or_2 (or_2_out, RES, demultiplexer_2_out0);
  or or_3 (or_3_out, RES, demultiplexer_3_out0);
  or or_4 (or_4_out, RES, demultiplexer_4_out0);
  or or_5 (or_5_out, RES, demultiplexer_5_out0);
  or or_6 (or_6_out, RES, demultiplexer_6_out0);
  or or_7 (or_7_out, RES, demultiplexer_7_out0);
  or or_8 (or_8_out, RES, demultiplexer_8_out0);
  LENGTH_CONTROL length_control_1 (
    .nACLK(nACLK), .Carry_In(nor_8_out), .W4015(W4015), .Dx(Dx), .Res(RES), .nLFO2(nLFO2), .nR4015(nR4015),
    .W400x(W400x), .NOSQA(NOxxx), .Dx_2(Dx_2), .STEP(length_control_1_step), .nACLK4(nACLK4));
  D_Flip_Flop #(.trigger("high")) d_ff_1 (
    .clk(length_control_1_step), .D(d_ff_9_qn), .Q(d_ff_1_q), .Qn(d_ff_1_qn), .preset(demultiplexer_1_out1),
    .reset(or_1_out));  // open: en
  not not_1 (not_1_out, HALT);
  D_Flip_Flop #(.trigger("high")) d_ff_2 (
    .clk(length_control_1_step), .D(d_ff_10_qn), .Q(d_ff_2_q), .Qn(d_ff_2_qn), .preset(demultiplexer_2_out1),
    .reset(or_2_out));  // open: en
  not not_2 (not_2_out, nor_1_out);
  D_Flip_Flop #(.trigger("high")) d_ff_3 (
    .clk(length_control_1_step), .D(d_ff_11_qn), .Q(d_ff_3_q), .Qn(d_ff_3_qn), .preset(demultiplexer_3_out1),
    .reset(or_3_out));  // open: en
  not not_3 (not_3_out, nor_2_out);
  D_Flip_Flop #(.trigger("high")) d_ff_4 (
    .clk(length_control_1_step), .D(d_ff_12_qn), .Q(d_ff_4_q), .Qn(d_ff_4_qn), .preset(demultiplexer_4_out1),
    .reset(or_4_out));  // open: en
  not not_4 (not_4_out, nor_3_out);
  D_Flip_Flop #(.trigger("high")) d_ff_5 (
    .clk(length_control_1_step), .D(d_ff_13_qn), .Q(d_ff_5_q), .Qn(d_ff_5_qn), .preset(demultiplexer_5_out1),
    .reset(or_5_out));  // open: en
  not not_5 (not_5_out, nor_4_out);
  D_Flip_Flop #(.trigger("high")) d_ff_6 (
    .clk(length_control_1_step), .D(d_ff_14_qn), .Q(d_ff_6_q), .Qn(d_ff_6_qn), .preset(demultiplexer_6_out1),
    .reset(or_6_out));  // open: en
  not not_6 (not_6_out, nor_5_out);
  D_Flip_Flop #(.trigger("high")) d_ff_7 (
    .clk(length_control_1_step), .D(d_ff_15_qn), .Q(d_ff_7_q), .Qn(d_ff_7_qn), .preset(demultiplexer_7_out1),
    .reset(or_7_out));  // open: en
  not not_7 (not_7_out, nor_6_out);
  D_Flip_Flop #(.trigger("high")) d_ff_8 (
    .clk(length_control_1_step), .D(d_ff_16_qn), .Q(d_ff_8_q), .Qn(d_ff_8_qn), .preset(demultiplexer_8_out1),
    .reset(or_8_out));  // open: en
  not not_8 (not_8_out, nor_7_out);
  xor xor_1 (xor_1_out, HALT, d_ff_1_qn);
  nor nor_1 (nor_1_out, not_1_out, d_ff_1_q);
  xor xor_2 (xor_2_out, nor_1_out, d_ff_2_qn);
  nor nor_2 (nor_2_out, not_2_out, d_ff_2_q);
  xor xor_3 (xor_3_out, nor_2_out, d_ff_3_qn);
  nor nor_3 (nor_3_out, not_3_out, d_ff_3_q);
  xor xor_4 (xor_4_out, nor_3_out, d_ff_4_qn);
  nor nor_4 (nor_4_out, not_4_out, d_ff_4_q);
  xor xor_5 (xor_5_out, nor_4_out, d_ff_5_qn);
  nor nor_5 (nor_5_out, not_5_out, d_ff_5_q);
  xor xor_6 (xor_6_out, nor_5_out, d_ff_6_qn);
  nor nor_6 (nor_6_out, not_6_out, d_ff_6_q);
  xor xor_7 (xor_7_out, nor_6_out, d_ff_7_qn);
  nor nor_7 (nor_7_out, not_7_out, d_ff_7_q);
  xor xor_8 (xor_8_out, nor_7_out, d_ff_8_qn);
  nor nor_8 (nor_8_out, not_8_out, d_ff_8_q);
  D_Flip_Flop #(.trigger("high")) d_ff_9 (.clk(nACLK), .D(xor_1_out), .Qn(d_ff_9_qn));  // open: Q, preset, en, reset
  D_Flip_Flop #(.trigger("high")) d_ff_10 (.clk(nACLK), .D(xor_2_out), .Qn(d_ff_10_qn));  // open: Q, preset, en, reset
  D_Flip_Flop #(.trigger("high")) d_ff_11 (.clk(nACLK), .D(xor_3_out), .Qn(d_ff_11_qn));  // open: Q, preset, en, reset
  D_Flip_Flop #(.trigger("high")) d_ff_12 (.clk(nACLK), .D(xor_4_out), .Qn(d_ff_12_qn));  // open: Q, preset, en, reset
  D_Flip_Flop #(.trigger("high")) d_ff_13 (.clk(nACLK), .D(xor_5_out), .Qn(d_ff_13_qn));  // open: Q, preset, en, reset
  D_Flip_Flop #(.trigger("high")) d_ff_14 (.clk(nACLK), .D(xor_6_out), .Qn(d_ff_14_qn));  // open: Q, preset, en, reset
  D_Flip_Flop #(.trigger("high")) d_ff_15 (.clk(nACLK), .D(xor_7_out), .Qn(d_ff_15_qn));  // open: Q, preset, en, reset
  D_Flip_Flop #(.trigger("high")) d_ff_16 (.clk(nACLK), .D(xor_8_out), .Qn(d_ff_16_qn));  // open: Q, preset, en, reset
endmodule

// LENGTH CONTROL
module LENGTH_CONTROL (
  input  nACLK4,
  input  nACLK,
  input  Carry_In,
  input  Dx,
  input  Res,
  input  W4015,
  input  nLFO2,
  input  W400x,
  input  nR4015,
  output STEP,
  output NOSQA,
  output Dx_2
);

  wire _5_out, _6_out, _7_out, _8_out, d_ff_1_qn, d_latch_1_q, d_latch_2_q, d_latch_3_q, not_1_out, not_2_out;

  not not_1 (not_1_out, nACLK);
  D_Flip_Flop #(.trigger("high")) d_ff_1 (
    .clk(not_1_out), .D(Dx), .Qn(d_ff_1_qn), .en(W4015), .reset(Res));  // open: Q, preset
  D_latch d_latch_1 (.EN(nACLK), .D(Carry_In), .Q(d_latch_1_q));  // open: NOT_Q
  D_latch d_latch_2 (.EN(nACLK), .D(d_ff_1_qn), .Q(d_latch_2_q));  // open: NOT_Q
  D_latch d_latch_3 (.EN(nACLK), .D(_5_out), .Q(d_latch_3_q));  // open: NOT_Q
  and _7 (_7_out, d_latch_1_q, STEP);
  and _8 (_8_out, nACLK4, d_latch_2_q);
  nor _4 (STEP, d_latch_3_q, nLFO2);
  nor _6 (_6_out, _7_out, _8_out, Res, _5_out);
  nor _5 (_5_out, _6_out, W400x);
  not not_2 (not_2_out, nR4015);
  not not_3 (NOSQA, _6_out);
  assign Dx_2 = not_2_out ? ~_5_out : 1'bz;  // Controlled_Inverter controlled_inverter_1

  // Notes on the sheet:
  //   DFF1
  //   3
  //   7
  //   8
  //   4
  //   R
  //   S
  //   Q
  //   1
  //   /Q
  //   9
  //   2
endmodule

// IO CONTROL
module IO_CONTROL (
  input  ACLK,
  input  nACLK,
  input  D0,
  input  D1,
  input  D2,
  input  W4016,
  input  nRES_PIN,
  input  [15:0] APU_Ax,
  input  R_W_int,
  input  nR4016,
  input  nR4017,
  input  DBG,
  input  nM2,
  input  nNMI_PIN,
  input  nIRQ_PIN,
  input  INT_from_apu,
  input  CLK_PIN,
  input  WR,
  input  [7:0] DB_IN_EXT,
  input  [7:0] DB_OUT,
  output OUT0_PIN,
  output OUT1_PIN,
  output OUT2_PIN,
  output MASTER_RESET,
  output [15:0] Ax,
  output R_W_PIN,
  output IN0_PIN,
  output IN1_PIN,
  output M2,
  output nNMI_INT,
  output nIRQ_INT,
  output nCLK_INT,
  output [7:0] DB_IN,
  output [7:0] DB_OUT_EXT
);

  wire d_ff_1_q, d_ff_2_q, d_ff_3_q, d_latch_1_q, d_latch_2_q, d_latch_3_q, nor_1_out, not_1_out, not_2_out,
       not_3_out, not_8_out, not_9_out, not_10_out, not_11_out, not_12_out, not_13_out;
  wire [7:0] nor_3_out;
  wire [7:7] not_4_out;

  not not_1 (not_1_out, ACLK);
  not not_2 (not_2_out, nACLK);
  not not_3 (not_3_out, R_W_int);
  not not_4 (not_4_out[7], not_3_out);
  D_Flip_Flop #(.trigger("high")) d_ff_1 (
    .clk(not_2_out), .D(D0), .Q(d_ff_1_q), .en(W4016));  // open: Qn, preset, reset
  D_Flip_Flop #(.trigger("high")) d_ff_2 (
    .clk(not_2_out), .D(D1), .Q(d_ff_2_q), .en(W4016));  // open: Qn, preset, reset
  D_Flip_Flop #(.trigger("high")) d_ff_3 (
    .clk(not_2_out), .D(D2), .Q(d_ff_3_q), .en(W4016));  // open: Qn, preset, reset
  not not_5 (MASTER_RESET, nRES_PIN);
  not not_6 (nNMI_INT, not_11_out);
  not not_7 (nCLK_INT, CLK_PIN);
  nor nor_1 (nor_1_out, nRES_PIN, DBG);
  not not_8 (not_8_out, nM2);
  nor nor_2 (nIRQ_INT, not_12_out, INT_from_apu);
  not not_9 (not_9_out, WR);
  assign OUT0_PIN = nRES_PIN ? d_latch_1_q : 1'bz;  // Controlled_Buffer controlled_buffer_1
  D_latch d_latch_1 (.EN(not_1_out), .D(d_ff_1_q), .Q(d_latch_1_q));  // open: NOT_Q
  assign OUT1_PIN = nRES_PIN ? d_latch_2_q : 1'bz;  // Controlled_Buffer controlled_buffer_2
  D_latch d_latch_2 (.EN(not_1_out), .D(d_ff_2_q), .Q(d_latch_2_q));  // open: NOT_Q
  assign OUT2_PIN = nRES_PIN ? d_latch_3_q : 1'bz;  // Controlled_Buffer controlled_buffer_3
  D_latch d_latch_3 (.EN(not_1_out), .D(d_ff_3_q), .Q(d_latch_3_q));  // open: NOT_Q
  assign Ax = nRES_PIN ? APU_Ax : 16'bz;  // Controlled_Buffer controlled_buffer_4
  assign R_W_PIN = nRES_PIN ? R_W_int : 1'bz;  // Controlled_Buffer controlled_buffer_5
  assign IN0_PIN = nRES_PIN ? nR4016 : 1'bz;  // Controlled_Buffer controlled_buffer_6
  assign IN1_PIN = nRES_PIN ? nR4017 : 1'bz;  // Controlled_Buffer controlled_buffer_7
  not not_10 (not_10_out, nor_1_out);
  assign M2 = not_10_out ? not_8_out : 1'bz;  // Controlled_Buffer controlled_buffer_8
  not not_11 (not_11_out, nNMI_PIN);
  not not_12 (not_12_out, nIRQ_PIN);
  assign DB_IN = not_9_out ? DB_IN_EXT : 8'bz;  // Controlled_Buffer controlled_buffer_9
  not not_13 (not_13_out, not_4_out[7]);
  assign nor_3_out = ~({8{not_4_out[7]}} | DB_OUT);  // NOR_Gate nor_3, 8 bits wide
  assign DB_OUT_EXT = not_13_out ? ~nor_3_out : 8'bz;  // Controlled_Inverter controlled_inverter_1

  // Notes on the sheet:
  //   /ACLK5
endmodule
