// Logisim project APUPlayer.circ as structural Verilog: 7 circuits, main circuit APUPlayer
module APUPlayer (
  input  nRES
);

  wire apu_dmc, apu_dmc_enirq, apu_dmc_loop, apu_nirq_cpu, apu_nnmi_cpu, apu_phi0__cpu, apu_r_w__ext,
       apu_rdy__cpu, apu_rmode, apu_rnd, apu_sqa, apu_sqb, apu_tri, comparator_1_eq, comparator_2_eq,
       core_phi1, core_phi2, core_r_w, Next_RegOp_out, not_1_out, XTAL_out;
  wire [1:0] apu_sqa_duty, apu_sqb_duty;
  wire [3:0] apu_dmcf, apu_n_req, transp_latch_3_q_2;
  wire [5:0] apu_n_env, apu_sqa_env, apu_sqb_env;
  wire [7:0] apu_aux_a, apu_db_out_ext, apu_sample_adr, apu_sample_buf, apu_sample_length, apu_sw_a,
       apu_sw_b, apu_tri_lin, core_db_out, counter_1_q, nes_memory_1_db_out, nes_memory_1_romout,
       transp_latch_q;
  wire [10:0] apu_sqa_f, apu_sqb_f, apu_tri_freq;
  wire [11:0] transp_latch_3_q;
  wire [14:0] apu_aux_b;
  wire [15:0] apu_ab, core_addr, transp_latch_2_q;
  wire [23:0] dumper_addr;
  wire [31:0] core_out_15, dumper_data;

  Clock XTAL (.out(XTAL_out));
  LED DMC (.in(apu_dmc));
  LED TRI (.in(apu_tri));
  LED SQB (.in(apu_sqb));
  LED SQA (.in(apu_sqa));
  LED RND (.in(apu_rnd));
  LED led_1 (.in(apu_tri_freq[0]));
  LED led_2 (.in(apu_tri_freq[1]));
  LED led_3 (.in(apu_tri_freq[2]));
  LED led_4 (.in(apu_tri_freq[3]));
  LED led_5 (.in(apu_tri_freq[4]));
  LED led_6 (.in(apu_tri_freq[5]));
  LED led_7 (.in(apu_tri_freq[6]));
  LED led_8 (.in(apu_tri_freq[7]));
  LED led_9 (.in(apu_tri_freq[8]));
  LED led_10 (.in(apu_tri_freq[9]));
  LED led_11 (.in(apu_tri_freq[10]));
  LED led_12 (.in(apu_tri_lin[0]));
  LED led_13 (.in(apu_tri_lin[1]));
  LED led_14 (.in(apu_tri_lin[2]));
  LED led_15 (.in(apu_tri_lin[3]));
  LED led_16 (.in(apu_tri_lin[4]));
  LED led_17 (.in(apu_tri_lin[5]));
  LED led_18 (.in(apu_tri_lin[6]));
  LED TRI_RELOAD (.in(apu_tri_lin[7]));
  _2A03_APU apu (
    .nRES_PIN(nRES), .RDY__CPU(apu_rdy__cpu), .R_W__CPU(core_r_w), .nIRQ_CPU(apu_nirq_cpu),
    .nNMI_CPU(apu_nnmi_cpu), .nNMI_PIN(1'b1), .R_W__EXT(apu_r_w__ext), .DBG__EXT(1'b0),
    .PHI0__CPU(apu_phi0__cpu), .nIRQ_PIN(1'b1), .Data_from_CPU(core_db_out), .AUX_A(apu_aux_a),
    .AUX_B(apu_aux_b), .CPU_Ax(core_addr), .AB(apu_ab), .DB_in_EXT(nes_memory_1_db_out),
    .DB_out_EXT(apu_db_out_ext), .PHI1_FromCore(core_phi1), .PHI2_FromCore(core_phi2), .CLK(XTAL_out),
    .RND(apu_rnd), .TRI(apu_tri), .SQB(apu_sqb), .SQA(apu_sqa), .DMC(apu_dmc), .SQA_F(apu_sqa_f),
    .SW_B(apu_sw_b), .SW_A(apu_sw_a), .SQB_F(apu_sqb_f), .N_ENV(apu_n_env), .RMODE(apu_rmode),
    .N_REQ(apu_n_req), .SQB_ENV(apu_sqb_env), .SQB_DUTY(apu_sqb_duty), .SQA_DUTY(apu_sqa_duty),
    .SQA_ENV(apu_sqa_env), .TRI_LIN(apu_tri_lin), .TRI_FREQ(apu_tri_freq), .DMCF(apu_dmcf),
    .DMC_ENIRQ(apu_dmc_enirq), .DMC_LOOP(apu_dmc_loop), .SAMPLE_LENGTH(apu_sample_length),
    .SAMPLE_BUF(apu_sample_buf), .SAMPLE_ADR(apu_sample_adr));  // open: OUT0, OUT1, OUT2, nIN0, nIN1, M2__EXT, Data_to_CPU
  LED led_19 (.in(apu_sqa_f[0]));
  LED led_20 (.in(apu_sqa_f[1]));
  LED led_21 (.in(apu_sqa_f[2]));
  LED led_22 (.in(apu_sqa_f[3]));
  LED led_23 (.in(apu_sqa_f[4]));
  LED led_24 (.in(apu_sqa_f[5]));
  LED led_25 (.in(apu_sqa_f[6]));
  LED led_26 (.in(apu_sqa_f[7]));
  LED led_27 (.in(apu_sqa_f[8]));
  LED led_28 (.in(apu_sqa_f[9]));
  LED led_29 (.in(apu_sqa_f[10]));
  LED SQA_ENV (.in(apu_sqa_env[0]));
  LED led_30 (.in(apu_sqa_env[1]));
  LED led_31 (.in(apu_sqa_env[2]));
  LED led_32 (.in(apu_sqa_env[3]));
  LED ENVDIS (.in(apu_sqa_env[4]));
  LED HALT_SQA (.in(apu_sqa_env[5]));
  LED SQA_DUTY (.in(apu_sqa_duty[0]));
  LED led_33 (.in(apu_sqa_duty[1]));
  LED led_34 (.in(apu_sw_a[0]));
  LED led_35 (.in(apu_sw_a[1]));
  LED led_36 (.in(apu_sw_a[2]));
  LED led_37 (.in(apu_sw_a[3]));
  LED led_38 (.in(apu_sw_a[4]));
  LED led_39 (.in(apu_sw_a[5]));
  LED led_40 (.in(apu_sw_a[6]));
  LED led_41 (.in(apu_sw_a[7]));
  LED led_42 (.in(apu_sqb_f[0]));
  LED led_43 (.in(apu_sqb_f[1]));
  LED led_44 (.in(apu_sqb_f[2]));
  LED led_45 (.in(apu_sqb_f[3]));
  LED led_46 (.in(apu_sqb_f[4]));
  LED led_47 (.in(apu_sqb_f[5]));
  LED led_48 (.in(apu_sqb_f[6]));
  LED led_49 (.in(apu_sqb_f[7]));
  LED led_50 (.in(apu_sqb_f[8]));
  LED led_51 (.in(apu_sqb_f[9]));
  LED led_52 (.in(apu_sqb_f[10]));
  LED SQB_ENV (.in(apu_sqb_env[0]));
  LED led_53 (.in(apu_sqb_env[1]));
  LED led_54 (.in(apu_sqb_env[2]));
  LED led_55 (.in(apu_sqb_env[3]));
  LED ENVDIS_2 (.in(apu_sqb_env[4]));
  LED HALT_SQB (.in(apu_sqb_env[5]));
  NES_MEMORY nes_memory_1 (
    .PH2(core_phi2), .Addr(apu_ab), .DB_in(apu_db_out_ext), .R_W(apu_r_w__ext), .nRES(nRES),
    .DB_out(nes_memory_1_db_out), .ROMout(nes_memory_1_romout));
  Fake6502 core (
    .PHI0(apu_phi0__cpu), .RDY(apu_rdy__cpu), .SO(1'b1), .nNMI(apu_nnmi_cpu), .nIRQ(apu_nirq_cpu),
    .nRES(nRES), .PHI1(core_phi1), .PHI2(core_phi2), .R_W(core_r_w), .Addr(core_addr), .DB_out(core_db_out),
    .out_15(core_out_15), .in_8(Next_RegOp_out));  // open: DB_in, SYNC
  LED SQB_DUTY (.in(apu_sqb_duty[0]));
  LED led_56 (.in(apu_sqb_duty[1]));
  LED led_57 (.in(apu_sw_b[0]));
  LED led_58 (.in(apu_sw_b[1]));
  LED led_59 (.in(apu_sw_b[2]));
  LED led_60 (.in(apu_sw_b[3]));
  LED led_61 (.in(apu_sw_b[4]));
  LED led_62 (.in(apu_sw_b[5]));
  LED led_63 (.in(apu_sw_b[6]));
  LED led_64 (.in(apu_sw_b[7]));
  Button Next_RegOp (.out(Next_RegOp_out));
  // Probe on core_out_15
  LED RMODE (.in(apu_rmode));
  LED NFREQ (.in(apu_n_req[0]));
  LED led_65 (.in(apu_n_req[1]));
  LED led_66 (.in(apu_n_req[2]));
  LED led_67 (.in(apu_n_req[3]));
  LED N_ENV (.in(apu_n_env[0]));
  LED led_68 (.in(apu_n_env[1]));
  LED led_69 (.in(apu_n_env[2]));
  LED led_70 (.in(apu_n_env[3]));
  LED ENVDIS_3 (.in(apu_n_env[4]));
  LED HALT_NOISE (.in(apu_n_env[5]));
  Hex_Digit_Display hex_digit_display_1 (.value(nes_memory_1_romout[7:4]));  // open: dp
  Hex_Digit_Display hex_digit_display_2 (.value(nes_memory_1_romout[3:0]));  // open: dp
  AUXDumper dumper (.PHI1(core_phi1), .AUX({1'b0, apu_aux_b, apu_aux_a}), .Addr(dumper_addr), .Data(dumper_data));
  LED SAMPLE_ADR (.in(apu_sample_adr[0]));
  LED led_71 (.in(apu_sample_adr[1]));
  LED led_72 (.in(apu_sample_adr[2]));
  LED led_73 (.in(apu_sample_adr[3]));
  LED led_74 (.in(apu_sample_adr[4]));
  LED led_75 (.in(apu_sample_adr[5]));
  LED led_76 (.in(apu_sample_adr[6]));
  LED led_77 (.in(apu_sample_adr[7]));
  LED SAMPLE_LEN (.in(apu_sample_length[0]));
  LED led_78 (.in(apu_sample_length[1]));
  LED led_79 (.in(apu_sample_length[2]));
  LED led_80 (.in(apu_sample_length[3]));
  LED led_81 (.in(apu_sample_length[4]));
  LED led_82 (.in(apu_sample_length[5]));
  LED led_83 (.in(apu_sample_length[6]));
  LED led_84 (.in(apu_sample_length[7]));
  Comparator #(.width(16)) comparator_1 (.a(16'h2004), .b(apu_ab), .eq(comparator_1_eq));  // open: gt, lt
  Comparator #(.width(16)) comparator_2 (.a(16'h4014), .b(apu_ab), .eq(comparator_2_eq));  // open: gt, lt
  Register #(.trigger("high")) transp_latch (.D(apu_db_out_ext), .Q(transp_latch_q), .clk(core_phi2));  // open: en, clr
  Counter counter_1 (
    .count(comparator_1_eq), .Q(counter_1_q), .clk(core_phi2), .clr(comparator_2_eq));  // open: load, D, carry
  Register #(.width(16), .trigger("high")) transp_latch_2 (
    .D(core_addr), .en(core_addr[14]), .Q(transp_latch_2_q), .clk(core_phi2));  // open: clr
  LED SAMPLE_BUF (.in(apu_sample_buf[0]));
  LED led_85 (.in(apu_sample_buf[1]));
  LED led_86 (.in(apu_sample_buf[2]));
  LED led_87 (.in(apu_sample_buf[3]));
  LED led_88 (.in(apu_sample_buf[4]));
  LED led_89 (.in(apu_sample_buf[5]));
  LED led_90 (.in(apu_sample_buf[6]));
  LED led_91 (.in(apu_sample_buf[7]));
  LED DMC_FREQ (.in(apu_dmcf[0]));
  LED led_92 (.in(apu_dmcf[1]));
  LED led_93 (.in(apu_dmcf[2]));
  LED led_94 (.in(apu_dmcf[3]));
  LED LOOP (.in(apu_dmc_loop));
  LED ENIRQ (.in(apu_dmc_enirq));
  not not_1 (not_1_out, comparator_1_eq);
  RAM ram_1 (.addr(counter_1_q), .data(transp_latch_q), .sel(comparator_1_eq), .clk(core_phi2), .ld(1'b0), .clr(1'b0));
  RAM #(.addrWidth(24), .dataWidth(32), .bus("asynch")) ram_2 (
    .addr(dumper_addr), .data(dumper_data), .sel(1'b1), .ld(1'b0), .clr(1'b0));
  Hex_Digit_Display hex_digit_display_3 (.value(transp_latch_3_q[11:8]));  // open: dp
  Hex_Digit_Display hex_digit_display_4 (.value(transp_latch_3_q_2));  // open: dp
  Register #(.width(16), .trigger("high")) transp_latch_3 (
    .D(apu_ab), .en(not_1_out), .Q({transp_latch_3_q_2, transp_latch_3_q}), .clk(core_phi2));  // open: clr
  Hex_Digit_Display hex_digit_display_5 (.value(transp_latch_2_q[15:12]));  // open: dp
  Hex_Digit_Display hex_digit_display_6 (.value(transp_latch_2_q[11:8]));  // open: dp
  Hex_Digit_Display hex_digit_display_7 (.value(transp_latch_3_q[7:4]));  // open: dp
  Hex_Digit_Display hex_digit_display_8 (.value(transp_latch_3_q[3:0]));  // open: dp
  Hex_Digit_Display hex_digit_display_9 (.value(transp_latch_2_q[3:0]));  // open: dp
  Hex_Digit_Display hex_digit_display_10 (.value(transp_latch_2_q[7:4]));  // open: dp

  // Notes on the sheet:
  //   TRI_F
  //   TRI_LIN
  //   SQA_F
  //   SW_A
  //   N.C.
  //   SQB_F
  //   SW_B
  //   Load regdump here
  //   Last READ  ROM BYTE
  //   OAM
  //   Taram-param-pam. Pam! Peep, peep, peep. Pipipipip, pip, pibibip
  //   SPRDMA ADDRESS
  //   Last APU Register
endmodule

module AUXDumper (
  input  PHI1,
  input  [23:0] AUX,
  output [23:0] Addr,
  output [31:0] Data
);

  wire adder_1_p3, and_1_out, counter_1_carry, counter_2_q, counter_3_q, multiplier_1_p3, s_r_ff_1_q;
  wire [31:0] aux_a_1_a, aux_b_1_a;

  AUX_A aux_a_1 (.d(AUX[7:0]), .a(aux_a_1_a));
  AUX_B aux_b_1 (.d(AUX[23:8]), .a(aux_b_1_a));
  and and_1 (and_1_out, PHI1, ~s_r_ff_1_q);  // AND_Gate
  Counter #(.width(23), .max('h7fffff), .ongoal("stay")) counter_1 (
    .Q(Addr[23:1]), .carry(counter_1_carry), .clk(and_1_out));  // open: load, D, count, clr
  // Multiplier multiplier_1: pin names not known; wires that end beside it: aux_a_1_a, 32'h3ecccccd, multiplier_1_p3
  Counter #(.width(1), .max('h1)) counter_2 (.Q(counter_2_q), .clk(and_1_out));  // open: load, D, count, carry, clr
  Counter #(.width(1), .max('h1), .trigger("falling")) counter_3 (
    .Q(counter_3_q), .clk(and_1_out));  // open: load, D, count, carry, clr
  // Adder adder_1: pin names not known; wires that end beside it: multiplier_1_p3, aux_b_1_a, adder_1_p3
  xnor xnor_1 (Addr[0], counter_2_q, counter_3_q);
  // Divider divider_1: pin names not known; wires that end beside it: adder_1_p3, 32'h40000000, Data
  S_R_Flip_Flop s_r_ff_1 (.S(counter_1_carry), .Q(s_r_ff_1_q));  // open: clk, R, Qn, preset, reset, en

  // Notes on the sheet:
  //   * 0.4
  //   float->uint32_t Convert: https://gregstoll.com/~gregstoll/floattohex/
  //   a + b
  //   The invention of the org to make the ADDR tick EVERY half cycle.
  //    : 2
  //   normalized samples in range [0.0f; 1.0f]
endmodule

module AUX_A (
  input  [7:0] d,
  output [31:0] a
);

  ROM #(.dataWidth(32)) rom_1 (.addr(d), .data(a), .sel(1'b1));

  // Notes on the sheet:
  //   0...255
  //   contents of rom_1 (hex, n*v repeats v):
  //   3ab77b8e 3d12a8ec 3d924925 3ddadec7 3e118b0c 3e3577e6 3e59364e 3e7cc69c 3e901495 3ea1af28 3eb33333
  //   3ec4a0e1 3ed5f85c 3ee739ce 3ef86563 3f04bda1 3d12a8ec 3d924925 3ddadec7 3e118b0c 3e3577e6 3e59364e
  //   3e7cc69c 3e901495 3ea1af28 3eb33333 3ec4a0e1 3ed5f85c 3ee739ce 3ef86563 3f04bda1 3f0d3dcb 3d924925
  //   3ddadec7 3e118b0c 3e3577e6 3e59364e 3e7cc69c 3e901495 3ea1af28 3eb33333 3ec4a0e1 3ed5f85c 3ee739ce
  //   3ef86563 3f04bda1 3f0d3dcb 3f15b343 3ddadec7 3e118b0c 3e3577e6 3e59364e 3e7cc69c 3e901495 3ea1af28
  //   3eb33333 3ec4a0e1 3ed5f85c 3ee739ce 3ef86563 3f04bda1 3f0d3dcb 3f15b343 3f1e1e1e 3e118b0c 3e3577e6
  //   3e59364e 3e7cc69c 3e901495 3ea1af28 3eb33333 3ec4a0e1 3ed5f85c 3ee739ce 3ef86563 3f04bda1 3f0d3dcb
  //   3f15b343 3f1e1e1e 3f267e6f 3e3577e6 3e59364e 3e7cc69c 3e901495 3ea1af28 3eb33333 3ec4a0e1 3ed5f85c
  //   3ee739ce 3ef86563 3f04bda1 3f0d3dcb 3f15b343 3f1e1e1e 3f267e6f 3f2ed44b 3e59364e 3e7cc69c 3e901495
  //   3ea1af28 3eb33333 3ec4a0e1 3ed5f85c 3ee739ce 3ef86563 3f04bda1 3f0d3dcb 3f15b343 3f1e1e1e 3f267e6f
  //   3f2ed44b 3f371fc4 3e7cc69c 3e901495 3ea1af28 3eb33333 3ec4a0e1 3ed5f85c 3ee739ce 3ef86563 3f04bda1
  //   3f0d3dcb 3f15b343 3f1e1e1e 3f267e6f 3f2ed44b 3f371fc4 3f3f60ef 3e901495 3ea1af28 3eb33333 3ec4a0e1
  //   3ed5f85c 3ee739ce 3ef86563 3f04bda1 3f0d3dcb 3f15b343 3f1e1e1e 3f267e6f 3f2ed44b 3f371fc4 3f3f60ef
  //   3f4797dd 3ea1af28 3eb33333 3ec4a0e1 3ed5f85c 3ee739ce 3ef86563 3f04bda1 3f0d3dcb 3f15b343 3f1e1e1e
  //   3f267e6f 3f2ed44b 3f371fc4 3f3f60ef 3f4797dd 3f4fc4a3 3eb33333 3ec4a0e1 3ed5f85c 3ee739ce 3ef86563
  //   3f04bda1 3f0d3dcb 3f15b343 3f1e1e1e 3f267e6f 3f2ed44b 3f371fc4 3f3f60ef 3f4797dd 3f4fc4a3 3f57e753
  //   3ec4a0e1 3ed5f85c 3ee739ce 3ef86563 3f04bda1 3f0d3dcb 3f15b343 3f1e1e1e 3f267e6f 3f2ed44b 3f371fc4
  //   3f3f60ef 3f4797dd 3f4fc4a3 3f57e753 3f600000 3ed5f85c 3ee739ce 3ef86563 3f04bda1 3f0d3dcb 3f15b343
  //   3f1e1e1e 3f267e6f 3f2ed44b 3f371fc4 3f3f60ef 3f4797dd 3f4fc4a3 3f57e753 3f600000 3f680ebc 3ee739ce
  //   3ef86563 3f04bda1 3f0d3dcb 3f15b343 3f1e1e1e 3f267e6f 3f2ed44b 3f371fc4 3f3f60ef 3f4797dd 3f4fc4a3
  //   3f57e753 3f600000 3f680ebc 3f701399 3ef86563 3f04bda1 3f0d3dcb 3f15b343 3f1e1e1e 3f267e6f 3f2ed44b
  //   3f371fc4 3f3f60ef 3f4797dd 3f4fc4a3 3f57e753 3f600000 3f680ebc 3f701399 3f780eaa 3f04bda1 3f0d3dcb
  //   3f15b343 3f1e1e1e 3f267e6f 3f2ed44b 3f371fc4 3f3f60ef 3f4797dd 3f4fc4a3 3f57e753 3f600000 3f680ebc
  //   3f701399 3f780eaa 3f800000
endmodule

module AUX_B (
  input  [15:0] d,
  output [31:0] a
);

  ROM #(.addrWidth(15), .dataWidth(32)) rom_1 (.addr(d[14:0]), .data(a), .sel(1'b1));

  // Notes on the sheet:
  //   0...32767
  //   contents of rom_1 (hex, n*v repeats v):
  //   39f0dbd4 3cc007b4 3d3f0e2a 3d8e915b 3dbd229a 3deb3ca3 3e0c709f 3e230913 3e39688b 3e4f8fdb 3e657fd7
  //   3e7b394d 3e885e84 3e9305e6 3e9d932f 3ea806be 3c40856f 3d0fa7f6 3d6e36ed 3da5e8fe 3dd43e69 3e010ec1
  //   3e17c406 3e2e3fe1 3e44832b 3e5a8eb7 3e706356 3e8300eb 3e8db57e 3e984fc8 3ea2d028 3ead36fd 3cc007b4
  //   3d3f0e2a 3d8e915b 3dbd229a 3deb3ca3 3e0c709f 3e230913 3e39688b 3e4f8fdb 3e657fd7 3e7b394d 3e885e84
  //   3e9305e6 3e9d932f 3ea806be 3eb260f0 3d0fa7f6 3d6e36ed 3da5e8fe 3dd43e69 3e010ec1 3e17c406 3e2e3fe1
  //   3e44832b 3e5a8eb7 3e706356 3e8300eb 3e8db57e 3e984fc8 3ea2d028 3ead36fd 3eb784a4 3d3f0e2a 3d8e915b
  //   3dbd229a 3deb3ca3 3e0c709f 3e230913 3e39688b 3e4f8fdb 3e657fd7 3e7b394d 3e885e84 3e9305e6 3e9d932f
  //   3ea806be 3eb260f0 3ebca222 3d6e36ed 3da5e8fe 3dd43e69 3e010ec1 3e17c406 3e2e3fe1 3e44832b 3e5a8eb7
  //   3e706356 3e8300eb 3e8db57e 3e984fc8 3ea2d028 3ead36fd 3eb784a4 3ec1b977 3d8e915b 3dbd229a 3deb3ca3
  //   3e0c709f 3e230913 3e39688b 3e4f8fdb 3e657fd7 3e7b394d 3e885e84 3e9305e6 3e9d932f 3ea806be 3eb260f0
  //   3ebca222 3ec6caae 3da5e8fe 3dd43e69 3e010ec1 3e17c406 3e2e3fe1 3e44832b 3e5a8eb7 3e706356 3e8300eb
  //   3e8db57e 3e984fc8 3ea2d028 3ead36fd 3eb784a4 3ec1b977 3ecbd5d1 3dbd229a 3deb3ca3 3e0c709f 3e230913
  //   3e39688b 3e4f8fdb 3e657fd7 3e7b394d 3e885e84 3e9305e6 3e9d932f 3ea806be 3eb260f0 3ebca222 3ec6caae
  //   3ed0daec 3dd43e69 3e010ec1 3e17c406 3e2e3fe1 3e44832b 3e5a8eb7 3e706356 3e8300eb 3e8db57e 3e984fc8
  //   3ea2d028 3ead36fd 3eb784a4 3ec1b977 3ecbd5d1 3ed5da09 3deb3ca3 3e0c709f 3e230913 3e39688b 3e4f8fdb
  //   3e657fd7 3e7b394d 3e885e84 3e9305e6 3e9d932f 3ea806be 3eb260f0 3ebca222 3ec6caae 3ed0daec 3edad333
  //   3e010ec1 3e17c406 3e2e3fe1 3e44832b 3e5a8eb7 3e706356 3e8300eb 3e8db57e 3e984fc8 3ea2d028 3ead36fd
  //   3eb784a4 3ec1b977 3ecbd5d1 3ed5da09 3edfc674 3e0c709f 3e230913 3e39688b 3e4f8fdb 3e657fd7 3e7b394d
  //   3e885e84 3e9305e6 3e9d932f 3ea806be 3eb260f0 3ebca222 3ec6caae 3ed0daec 3edad333 3ee4b3d8 3e17c406
  //   3e2e3fe1 3e44832b 3e5a8eb7 3e706356 3e8300eb 3e8db57e 3e984fc8 3ea2d028 3ead36fd 3eb784a4 3ec1b977
  //   3ecbd5d1 3ed5da09 3edfc674 3ee99b68 3e230913 3e39688b 3e4f8fdb 3e657fd7 3e7b394d 3e885e84 3e9305e6
  //   3e9d932f 3ea806be 3eb260f0 3ebca222 3ec6caae 3ed0daec 3edad333 3ee4b3d8 3eee7d2e 3e2e3fe1 3e44832b
  //   3e5a8eb7 3e706356 3e8300eb 3e8db57e 3e984fc8 3ea2d028 3ead36fd 3eb784a4 3ec1b977 3ecbd5d1 3ed5da09
  //   3edfc674 3ee99b68 3ef35936 3bc0c48a 3cefbb5a 3d56aa32 3d9a40f1 3dc8b438 3df6b0bb 3e121c1f 3e28a641
  //   3e3ef79a 3e551102 3e6af34a 3e804f9f 3e8b0ad4 3e95aba7 3ea03278 3eaa9fa7 3c9034de 3d2762c6 3d82da35
  //   3db1898a 3ddfc135 3e06c180 3e1d6856 3e33d5f9 3e4a0b3f 3e6008fd 3e75d001 3e85b08c 3e905e84 3e9af24a
  //   3ea56c3e 3eafccbf 3cefbb5a 3d56aa32 3d9a40f1 3dc8b438 3df6b0bb 3e121c1f 3e28a641 3e3ef79a 3e551102
  //   3e6af34a 3e804f9f 3e8b0ad4 3e95aba7 3ea03278 3eaa9fa7 3eb4f391 3d2762c6 3d82da35 3db1898a 3ddfc135
  //   3e06c180 3e1d6856 3e33d5f9 3e4a0b3f 3e6008fd 3e75d001 3e85b08c 3e905e84 3e9af24a 3ea56c3e 3eafccbf
  //   3eba1429 3d56aa32 3d9a40f1 3dc8b438 3df6b0bb 3e121c1f 3e28a641 3e3ef79a 3e551102 3e6af34a 3e804f9f
  //   3e8b0ad4 3e95aba7 3ea03278 3eaa9fa7 3eb4f391 3ebf2e91 3d82da35 3db1898a 3ddfc135 3e06c180 3e1d6856
  //   3e33d5f9 3e4a0b3f 3e6008fd 3e75d001 3e85b08c 3e905e84 3e9af24a 3ea56c3e 3eafccbf 3eba1429 3ec442d6
  //   3d9a40f1 3dc8b438 3df6b0bb 3e121c1f 3e28a641 3e3ef79a 3e551102 3e6af34a 3e804f9f 3e8b0ad4 3e95aba7
  //   3ea03278 3eaa9fa7 3eb4f391 3ebf2e91 3ec95101 3db1898a 3ddfc135 3e06c180 3e1d6856 3e33d5f9 3e4a0b3f
  //   3e6008fd 3e75d001 3e85b08c 3e905e84 3e9af24a 3ea56c3e 3eafccbf 3eba1429 3ec442d6 3ece591f 3dc8b438
  //   3df6b0bb 3e121c1f 3e28a641 3e3ef79a 3e551102 3e6af34a 3e804f9f 3e8b0ad4 3e95aba7 3ea03278 3eaa9fa7
  //   3eb4f391 3ebf2e91 3ec95101 3ed35b39 3ddfc135 3e06c180 3e1d6856 3e33d5f9 3e4a0b3f 3e6008fd 3e75d001
  //   3e85b08c 3e905e84 3e9af24a 3ea56c3e 3eafccbf 3eba1429 3ec442d6 3ece591f 3ed8575b 3df6b0bb 3e121c1f
  //   3e28a641 3e3ef79a 3e551102 3e6af34a 3e804f9f 3e8b0ad4 3e95aba7 3ea03278 3eaa9fa7 3eb4f391 3ebf2e91
  //   3ec95101 3ed35b39 3edd4d90 3e06c180 3e1d6856 3e33d5f9 3e4a0b3f 3e6008fd 3e75d001 3e85b08c 3e905e84
  //   3e9af24a 3ea56c3e 3eafccbf 3eba1429 3ec4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
endmodule

module Fake6502 (
  input  PHI0,
  input  SO,
  input  nNMI,
  input  nIRQ,
  input  nRES,
  input  [7:0] DB_in,
  input  RDY,
  input  in_8,
  output PHI1,
  output PHI2,
  output R_W,
  output SYNC,
  output [15:0] Addr,
  output [7:0] DB_out,
  output [31:0] out_15
);

  wire [23:0] redump_redump_addr;
  wire [31:0] rom_1_data;

  ROM #(.addrWidth(24), .dataWidth(32)) rom_1 (.addr(redump_redump_addr), .data(rom_1_data), .sel(1'b1));
  RegDumpProcessor redump (
    .PHI0(PHI0), .regdump_data(rom_1_data), .Core_R_W(R_W), .Core_AB(Addr), .Core_DB(DB_out),
    .redump_addr(redump_redump_addr), .out_9(out_15), .in_2(in_8), .RDY(RDY));
  not not_1 (PHI1, PHI0);

  assign PHI2 = PHI0;
  assign SYNC = 1'b0;

  // Notes on the sheet:
  //   N.C.
  //   N.C.
  //   N.C.
  //   Load regdump here
  //   contents of rom_1 (hex, n*v repeats v):
  //   101 1000 8 801 103 c10 a 3411 a c012 a 3f13 b f15 7 1f15 63cb 8214 4fc 116 6 16 1b3 116 6 16 35d
  //   800c 8 80d 15 80f 8 e 136 ff08 8 809 15 90b 8 7d0a e6 7604 8 805 14 ab06 af 1000 8 801 6703 214 4fc
  //   116 6 16 1b3 116 6 16 2fd 800c 8 80d 13e ff08 8 809 15 90b 8 930a e6 7904 8 805 14 ab06 af 1000 8
  //   801 6778 214 4fc 116 6 16 1b3 116 6 16 2fd 800c 8 80d 10e 8 8 809 ee 7804 8 805 14 ab06 af 1000 8
  //   801 67bd 214 4fc 116 6 16 1b3 116 6 16 2fd 800c 8 80d ea 8 8 809 10f 7804 8 805 14 ab06 af 1000 8
  //   801 67c1 214 4f9 116 6 16 1b6 116 6 16 2f9 800c b 80d 103 8 8 809 106 7104 8 805 14 ab06 af 1000 8
  //   801 67b2 214 4f9 116 6 16 1b7 116 6 16 2fd 800c 8 80d b7 8 8 809 ee 7504 8 805 14 ab06 af 1000 8 801
  //   6815 214 4f9 116 6 16 1b6 116 6 16 2fd 800c 8 80d b7 8 8 809 ee 7404 8 805 14 ab06 af 1000 b 801
  //   6811 214 4f8 116 6 16 1b6 116 6 16 2fd 800c 8 80d b7 8 8 809 111 7304 8 805 14 ac06 b3 1000 8 801
  //   67f0 214 4fc 116 6 16 1b3 116 6 16 2fd 800c 8 80d b7 8 8 809 115 7204 8 805 14 ae06 af 1000 8 801
  //   67ed 214 4fc 116 6 16 1b3 116 6 16 35d 800c 8 80d 15 80f 8 30e 136 ff08 8 809 15 90b 8 670a 174 7404
  //   8 805 15 907 8 6706 af 1000 8 801 12d c10 a 3411 a c012 a 3f13 b f15 7 1f15 650f 214 4fb 116 6 16
  //   1b3 116 6 16 35d 800c 8 80d 15 80f 8 e 136 ff08 8 809 15 90b 8 7d0a e6 7604 8 805 14 6706 af 1000 8
  //   801 6703 214 4fb 116 6 16 1b3 116 6 16 2fd 800c 8 80d 13e ff08 8 809 15 90b 8 930a e6 7904 8 805 14
  //   6706 af 1000 8 801 677f 214 4f9 116 6 16 1b7 116 6 16 2f9 800c 8 80d 10e 8 8 809 ee 7804 8 805 14
  //   6706 af 1000 8 801 67bb 214 4fa 116 6 16 1b7 116 6 16 2fd 800c 8 80d f0 8 8 809 10f 7804 8 805 14
  //   6706 af 1000 8 801 67bb 214 4f9 116 6 16 1b7 116 6 16 2fd 800c 8 80d f0 8 8 809 106 7104 8 805 14
  //   6706 b3 1000 8 801 67bd 214 4fa 116 6 16 1b7 116 6 16 2fd 800c 8 80d b7 8 8 809 ee 7504 8 805 14
  //   6706 b3 1000 8 801 680e 214 4f8 116 6 16 1b7 116 6 16 2fd 800c 8 80d b7 8 8 809 ee 7404 8 805 14
  //   6706 b3 1000 8 801 6811 214 4fb 116 6 16 1b3 116 6 16 2fd 800c 8 80d b7 8 8 809 115 7304 8 805 14
  //   6806 af 1000 8 801 67f0 214 4fb 116 6 16 1b3 116 6 16 2fd 800c 8 80d b7 8 8 809 115 7204 8 805 14
  //   6a06 af 1000 8 801 67ed 214 4fc 116 6 16 1b3 116 6 16 3a3 810c 8 80d 19 80f 8 790e 12c ff08 8 809 15
  //   80b 8 fe0a 174 7404 8 805 15 907 8 ab06 250 7300 8 801 15 903 8 ab02 121 c10 a 3411 e c012 a 3f13 b
  //   f15 7 1f15 6319 214 4fc 116 6 16 1b3 116 6 16 361 810c 8 80d 15 80f 8 30e 12c ff08 8 809 15 90b 8
  //   d0a e6 7604 8 805 14 ab06 b9 7300 8 801 6701 214 4fa 116 6 16 1b7 116 6 16 2fd 810c 8 80d 134 ff08 8
  //   809 15 90b 8 1d0a e6 7904 8 805 14 ab06 b9 7300 8 801 6776 214 4fa 116 6 16 1b7 116 6 16 2fd 810c 8
  //   80d 134 ff08 8 809 15 90b 8 2e0a e6 7804 8 805 14 ab06 bd 7300 8 801 6772 214 4fa 116 6 16 1b7 116 6
  //   16 2fd 810c 8 80d 134 ff08 8 809 15 90b 8 400a 107 7804 8 805 18 ab06 b9 7300 8 801 6751 214 4f8 116
  //   6 16 1b7 116 6 16 2fd 810c 8 80d 134 ff08 8 809 15 90b 8 530a 102 7104 8 805 14 ab06 b9 7300 8 801
  //   675d 214 4fb 116 6 16 1b3 116 6 16 2fd 810c 8 80d 134 ff08 8 809 15 90b 8 670a ea 7504 8 805 14 ab06
  //   b9 7300 8 801 6775 214 4fa 116 6 16 1b3 116 6 16 2fc 810c 8 80d 134 ff08 8 809 19 90b 8 7d0a e6 7404
  //   8 805 14 ab06 b9 7300 8 801 6778 214 4fc 116 6 16 1b3 116 6 16 2fd 810c 8 80d 138 ff08 8 809 15 90b
  //   8 930a 109 7304 8 805 14 ac06 b9 7300 8 801 6753 214 4fc 116 6 16 1b3 116 6 16 2fd 810c 8 80d 108 8
  //   8 809 111 7204 8 805 14 ae06 b9 7300 8 801 6797 214 4f9 116 6 16 1b7 116 6 16 3a3 800c 8 80d 15 80f
  //   8 30e 1f3 ff08 8 809 15 90b 8 670a 19e 7404 8 805 15 907 8 4006 132 7300 8 801 15 903 8 6702 125 c10
  //   a 3411 a c012 a 3f13 b f15 7 1f15 6347 214 4f9 116 6 16 1b7 116 6 16 35d 800c 8 80d 15 80f 8 e 132
  //   ff08 8 809 15 90b 8 7d0a 159 7604 8 805 15 907 8 2e06 b9 7300 8 801 667f 214 4fa 116 6 16 1b7 116 6
  //   16 2fd 800c 8 80d 13a ff08 8 809 15 90b 8 930a ed 7904 8 805 14 2e06 bd 7300 8 801 6769 214 4fa 116
  //   6 16 1b6 116 6 16 2fd 800c 8 80d 10a 8 8 809 15d 7804 8 805 15 907 8 1d06 b9 7300 8 801 673c 214 4fc
  //   116 6 16 1b3 116 6 16 2fd 800c 8 80d f0 8 8 809 113 7804 8 805 14 1d06 b9 7300 8 801 67ae 214 4fc
  //   116 6 16 1b3 116 6 16 2fd 800c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
endmodule

module NES_MEMORY (
  input  nRES,
  input  PH2,
  input  [7:0] DB_in,
  input  [15:0] Addr,
  input  R_W,
  output [7:0] DB_out,
  output [7:0] ROMout
);

  wire and_1_out, and_2_out, nor_1_out, not_1_out, not_2_out;
  wire [7:0] ram_1_data, rom_1_data;

  nor nor_1 (nor_1_out, Addr[13], Addr[14]);
  and and_1 (and_1_out, PH2, nor_1_out);
  and and_2 (and_2_out, PH2, Addr[15]);
  not not_1 (not_1_out, R_W);
  RAM #(.addrWidth(11), .bus("separate")) ram_1 (
    .addr(Addr[10:0]), .din(DB_in), .data(ram_1_data), .str(not_1_out), .sel(and_1_out), .clk(and_1_out),
    .ld(R_W), .clr(not_2_out));
  not not_2 (not_2_out, nRES);
  ROM #(.addrWidth(16)) rom_1 (.addr(Addr), .data(rom_1_data), .sel(and_2_out));
  assign DB_out = and_1_out ? ram_1_data : 8'bz;  // Controlled_Buffer controlled_buffer_1
  assign DB_out = R_W ? rom_1_data : 8'bz;  // Controlled_Buffer controlled_buffer_2
  Register #(.trigger("falling")) register_1 (.D(rom_1_data), .en(R_W), .Q(ROMout), .clk(PH2));  // open: clr

  // Notes on the sheet:
  //   WRAM
  //   Load 64K CPU Memory dump here (with DPCM samples)
  //   PRG ROM
  //   contents of rom_1 (hex, n*v repeats v):
  //   0 8f 0 98 d8 2 8 7*0 23 0 b 0 b 70 0 0 a0 a0 165*0 3 20*0 1 0 1 11*0 80 4 b1 5 b2 1f 8 fc 1 0 80 6*0
  //   1 1 0 0 0 1 3 0 55 24 0 0 0 1e b0 0 ff f6 3 b8 c8 d8 23 16 3 b9 c9 d9 23 36 3 ba ca da 23 56 3 bb cb
  //   db ff 58*0 ff 17*0 9c 2a 24*0 20 10 0 20 20 26 10 15 20 0 10 f 20 0 10 f 20 0 10 f 20 0 10 f 20 2c
  //   3c 21 5*20 10 0 20 20 26 10 15 20 0 10 f 5*20 0 10 f 20 0 10 f 8*20 48*0 57 57 c8 57 c8 0 d1 c1 55
  //   24 b8 c8 33 b4 a5 c0 f0 b9 1 b0 f0 c9 1 b8 f0 d9 1 c0 f0 bb 1 b0 f0 cb 1 b8 f0 db 1 c0 f0 39 0 c0 f0
  //   49 0 c8 f0 59 0 d0 f0 69 0 d8 f0 2b 0 b8 f0 3b 0 c0 f0 4b 0 c8 f0 5b 0 d0 f0 6b 0 d8 40 39 0 c0 40
  //   49 0 c8 40 59 0 d0 40 69 0 d8 50 2b 0 b8 50 3b 0 c0 50 4b 0 c8 50 5b 0 d0 50 6b 0 d8 a0 b7 2 a0 a0
  //   c7 2 a8 a0 d7 2 b0 a0 e7 2 b8 a0 f7 2 c0 90 c5 2 a8 90 d5 2 b0 90 e5 2 b8 90 f5 2 c0 80 f3 2 c0 88
  //   b1 2 c8 88 c1 2 d0 88 d1 2 d8 98 b3 2 c8 98 c3 2 d0 f0 0 0 0 f0 0 0 0 f0 0 0 0 f0 0 0 0 f0 0 0 0 f0
  //   0 0 0 f0 0 0 0 f0 0 0 0 f0 0 0 0 f0 0 0 0 f0 0 0 0 f0 0 0 0 f0 0 0 0 f0 0 0 0 f0 0 0 0 f0 0 0 0 f0 0
  //   0 0 f0 0 0 0 f0 0 0 0 f0 0 0 0 f0 0 0 0 f0 0 0 0 f0 0 0 0 f0 0 0 0 f0 5*0 5 1023*0 88 88 80 80 4*0
  //   63 3e 3e aa 4*0 ab aa ad af 5*0 1 2 3 4*0 32 32 1 1 12*0 56 41 ab e8 6*0 ad af 4*0 1 1 2 2 12*0 5 5
  //   6*0 5 5 14*0 fc ab 67 3 4*0 1 1 1 5*0 4*80 4*0 51 42 ff 80 4*0 b2 b2 6*0 2 2 1 1 4*0 34 74 ff 80 4*0
  //   f f 6*0 9 9 6*0 fb fb 8 8 4*0 97 97 14*0 8 8 6*0 7 7 6*0 80 0 5 0 b1 0 5 0 a 0 a 0 1a 0 b1 5*0 80
  //   30737*0 70 80 7c 80 86 80 8b 80 90 80 95 80 a1 80 b3 80 b8 80 d1 80 df 80 ed 80 2 81 7 81 14 81 19
  //   81 1e 81 28 81 38 81 47 81 56 81 5f 81 69 81 6e 81 77 81 93 81 94 81 a8 81 bc 81 d0 81 ec 81 0 82 30
  //   82 41 82 55 82 64 82 1c 82 73 82 85 82 7c 82 94 82 a7 82 ba 82 cd 82 db 82 e9 82 f3 82 ff 82 30 82
  //   13 83 22 83 31 83 43 83 57 83 6f 83 74 83 20 9e 84 a9 e 85 d3 a9 0 4c 7d 83 a9 1 20 7d 83 a9 10 4c
  //   da 84 a9 2 4c 7d 83 a9 3 4c 7d 83 a9 4 4c 7d 83 20 9e 84 a9 d 85 d3 a9 5 4c 7d 83 a5 13 18 69 f0 85
  //   13 a5 12 69 ff 85 12 a9 6 4c 7d 83 a9 7 4c 7d 83 20 9e 84 a9 c 85 d3 a9 0 85 1c a9 8 20 7d 83 a9 80
  //   85 13 a9 0 4c da 84 a9 9 85 d3 a9 9 20 7d 83 a9 2 4c da 84 a9 a 20 7d 83 a9 20 85 1b a9 4 4c da 84
  //   a9 b 20 7d 83 a9 80 85 11 20 f1 84 85 1c 29 3 85 1a 85 1d 60 a9 c 4c 7d 83 a9 80 85 13 a9 10 85 1c
  //   a9 d 4c 7d 83 a9 e 4c 7d 83 a9 f 4c 7d 83 a9 10 20 7d 83 a9 20 4c da 84 a9 11 20 7d 83 a5 12 85 1b
  //   a5 19 9 8 85 19 60 a9 12 20 7d 83 a9 80 85 13 20 f1 84 85 1a 60 a9 80 85 13 c6 12 a9 10 85 1c a9 13
  //   4c 7d 83 a9 80 85 1c a9 14 4c 7d 83 a9 15 20 7d 83 a9 20 4c da 84 a9 16 4c 7d 83 a9 80 85 13 a9 17
  //   4c 7d 83 a9 18 20 7d 83 a9 2c 85 1c a9 20 85 1d a9 f0 85 1e a9 90 85 11 a5 19 9 8 85 19 60 60 a9 1a
  //   20 7d 83 a9 1c 85 1c a9 10 85 1d a9 f0 85 1e 4c 88 81 a9 1b 20 7d 83 a9 b 85 1c a9 0 85 1d a9 f0 85
  //   1e 4c e1 81 a9 1c 20 7d 83 a9 1c 85 1c a9 10 85 1d a9 10 85 1e 4c e1 81 a9 1d 20 7d 83 a9 3b 85 1c
  //   a9 30 85 1d a9 f0 85 1e a9 90 85 11 a5 19 9 8 85 19 60 a9 1e 20 7d 83 a9 19 85 1c a9 10 85 1d a9 10
  //   85 1e 4c 11 82 a9 1f 20 7d 83 a9 2b 85 1c a9 20 85 1d a9 f0 85 1e a9 90 85 11 a5 19 9 8 85 19 60 a9
  //   20 20 7d 83 a9 2a 85 1c a9 20 85 1d a9 10 85 1e 4c 11 82 a9 80 85 11 c6 10 a5 19 9 8 85 19 a9 23 4c
  //   7d 83 a9 10 85 11 a5 19 9 8 85 19 a9 24 20 7d 83 a9 10 85 15 60 a9 0 85 16 a5 19 9 8 85 19 a9 25 4c
  //   7d 83 a9 0 85 16 a5 19 9 8 85 19 a9 26 4c 7d 83 a9 80 85 13 a9 27 4c 7d 83 a9 80 85 13 a9 28 4c 7d
  //   83 a9 0 85 16 a5 19 9 8 85 19 a9 29 4c 7d 83 a9 5 85 1c a9 40 85 1d a5 19 9 8 85 19 a9 2a 4c 7d 83
  //   a9 3 85 1c a9 30 85 1d a5 19 9 8 85 19 a9 2b 4c 7d 83 a9 4 85 1c a9 28 85 1d a5 19 9 8 85 19 a9 2c
  //   4c 7d 83 a9 2d 20 7d 83 a9 83 85 1d a9 8 85 1b 60 a9 2e 20 7d 83 a9 10 85 1d a9 20 4c da 84 a9 2f 20
  //   7d 83 a9 4 4c da 84 20 9e 84 a9 f 85 d3 a9 30 4c 7d 83 a9 31 20 7d 83 a9 80 85 11 a5 12 85 1b a5 19
  //   9 8 85 19 60 a9 0 85 16 a5 19 9 8 85 19 a9 32 4c 7d 83 a9 0 85 16 a5 19 9 8 85 19 a9 33 4c 7d 83 a9
  //   34 20 7d 83 a5 12 85 1b c6 1b a5 19 9 8 85 19 60 a9 35 20 7d 83 a9 80 85 11 a5 12 85 1b a5 19 9 8 85
  //   19 60 a9 36 20 7d 83 a9 20 85 15 a9 80 85 11 a5 12 85 1b a5 19 9 8 85 19 60 a9 38 4c 7d 83 a9 80 85
  //   13 a9 39 4c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
endmodule

module RegDumpProcessor (
  input  PHI0,
  input  in_2,
  input  [31:0] regdump_data,
  input  RDY,
  output Core_R_W,
  output [15:0] Core_AB,
  output [7:0] Core_DB,
  output [23:0] redump_addr,
  output [31:0] out_9
);

  wire and_1_out, and_2_out, cnt_ovf_reg_q, comparator_1_eq, comparator_1_gt, comparator_2_eq,
       comparator_3_gt, multiplexer_1_out, multiplexer_2_out, not_1_out, or_1_out, or_2_out, or_3_out;
  wire [7:0] regop_word_q_2, undriven;
  wire [15:0] or_4_out;
  wire [31:0] delta_phi_word_q, multiplexer_3_out, multiplexer_4_out, regop_word_q, subtractor_1_out;

  or or_1 (or_1_out, in_2, cnt_ovf_reg_q);
  Multiplexer #(.enable("false")) multiplexer_1 (.in0(1'b1), .in1(1'b1), .out(multiplexer_1_out), .sel(or_1_out));
  Multiplexer #(.enable("false")) multiplexer_2 (.in0(1'b1), .in1(1'b0), .out(multiplexer_2_out), .sel(or_1_out));
  Multiplexer #(.width(32), .enable("false")) multiplexer_3 (
    .in0(regdump_data), .in1(32'h20), .out(multiplexer_3_out), .sel(in_2));
  Register #(.width(32)) delta_phi_word (.D(regdump_data), .Q(delta_phi_word_q), .clk(cnt_ovf_reg_q));  // open: en, clr
  or or_2 (or_2_out, comparator_1_gt, comparator_1_eq);
  Comparator #(.width(32)) comparator_1 (
    .a(regdump_data), .b(32'h2), .gt(comparator_1_gt), .eq(comparator_1_eq));  // open: lt
  Subtractor #(.width(32)) subtractor_1 (.a(regdump_data), .b(32'h2), .out(subtractor_1_out));  // open: bin, bout
  Counter #(.width(32), .max('hffffffff), .ongoal("stay")) phi_dec_cnt (
    .load(multiplexer_1_out), .D(multiplexer_3_out), .count(multiplexer_2_out), .Q(out_9), .clk(PHI0));  // open: carry, clr
  Multiplexer #(.width(32), .enable("false")) multiplexer_4 (
    .in0(32'h1), .in1(subtractor_1_out), .out(multiplexer_4_out), .sel(or_2_out));
  Register #(.width(32)) regop_word (
    .D(regdump_data), .Q({regop_word_q[31:16], regop_word_q_2, regop_word_q[7:0]}), .clk(and_1_out),
    .clr(cnt_ovf_reg_q));  // open: en
  Comparator #(.width(32)) comparator_2 (.a(out_9), .b({32{1'b0}}), .eq(comparator_2_eq));  // open: gt, lt
  Comparator #(.width(32)) comparator_3 (.a(delta_phi_word_q), .b({32{1'b0}}), .gt(comparator_3_gt));  // open: eq, lt
  Register #(.width(1)) cnt_ovf_reg (.D(comparator_2_eq), .Q(cnt_ovf_reg_q), .clk(PHI0));  // open: en, clr
  and and_1 (and_1_out, PHI0, comparator_3_gt, comparator_2_eq, ~cnt_ovf_reg_q);  // AND_Gate
  or or_3 (or_3_out, and_1_out, cnt_ovf_reg_q);
  assign or_4_out = 16'h4000 | {{11{1'b0}}, regop_word_q[4:0]};  // OR_Gate or_4, 16 bits wide
  not not_1 (not_1_out, regop_word_q[7]);
  Multiplexer #(.enable("false")) multiplexer_5 (.in0(1'b1), .in1(regop_word_q[7]), .out(Core_R_W), .sel(and_1_out));
  Multiplexer #(.width(16), .enable("false")) multiplexer_6 (
    .in0({16{1'b0}}), .in1(or_4_out), .out(Core_AB), .sel(and_1_out));
  Multiplexer #(.width(8), .enable("false")) multiplexer_7 (
    .in0(undriven), .in1(regop_word_q_2), .out(Core_DB), .sel(and_2_out));
  and and_2 (and_2_out, and_1_out, not_1_out, RDY);
  Counter #(.width(24), .max('hffffff), .ongoal("stay"), .trigger("falling")) addr_cnt (
    .load(1'b0), .count(1'b1), .Q(redump_addr), .clk(or_3_out));  // open: D, carry, clr

  // Notes on the sheet:
  //   https://github.com/emu-russia/breaknes/blob/main/BreaksAPU/NSFPlayerInterop/RegDumpProcessor.cpp
  //   Load/Decrement Setup (1: Load; 0: Decrement)
  //   Do RegOp
  //   Load PHI Counter
  //   RegOp Setup
  //   Reg Index (0-0x1f)
  //   Reg Address
  //   Value (if write)
  //   1: Read register
  //   Default: Read address 0x0000
  //   1: RegOp + Write
  //   Falling edge
endmodule
