// Logisim project APUPlayerEvo.circ as structural Verilog: 7 circuits, main circuit APUPlayer
module APUPlayer (
  input  n_RES
);

  wire apu_m2, apu_n_in0, apu_n_in1, apu_n_irq_tocore, apu_out_0, apu_out_1, apu_out_2, apu_phi0_tocore,
       apu_rdy_tocore, apu_rnw, core_phi1, core_phi2, core_rnw, Next_RegOp_out, XTAL_out;
  wire [3:0] transp_latch_q_2, transp_latch_q_3;
  wire [7:0] apu_aux_a, apu_d_out, apu_db_tocore, core_db_out, transp_latch_q, wram_1_db_out;
  wire [14:0] apu_aux_b;
  wire [15:0] apu_ax, core_addr;
  wire [23:0] dumper_addr;
  wire [31:0] aux_dump_dout, core_counter, dumper_data;

  Clock XTAL (.out(XTAL_out));
  APU_NoCore apu (
    .CLK(XTAL_out), .n_RES(n_RES), .n_IRQ(1'b1), .PHI1_FromCore(core_phi1), .PHI2_FromCore(core_phi2),
    .Addr_FromCore(core_addr), .DB_FromCore(core_db_out), .RnW_FromCore(core_rnw), .DBG(1'b0),
    .D_In(wram_1_db_out), .PHI0_ToCore(apu_phi0_tocore), .M2(apu_m2), .RnW(apu_rnw), .n_IN0(apu_n_in0),
    .n_IN1(apu_n_in1), .OUT_0(apu_out_0), .OUT_1(apu_out_1), .OUT_2(apu_out_2), .RDY_ToCore(apu_rdy_tocore),
    .n_IRQ_ToCore(apu_n_irq_tocore), .Ax(apu_ax), .DB_ToCore(apu_db_tocore), .D_Out(apu_d_out),
    .AUX_A(apu_aux_a), .AUX_B(apu_aux_b));
  // NoConnect on apu_n_in0
  // NoConnect on apu_n_in1
  // NoConnect on apu_out_0
  // NoConnect on apu_out_1
  // NoConnect on apu_out_2
  WRAM wram_1 (.Addr(apu_ax), .DB_in(apu_d_out), .RnW(apu_rnw), .n_RES(n_RES), .M2(apu_m2), .DB_out(wram_1_db_out));
  Fake6502 core (
    .RDY(apu_rdy_tocore), .SO(1'b1), .n_NMI(1'b1), .n_IRQ(apu_n_irq_tocore), .n_RES(n_RES),
    .DB_in(apu_db_tocore), .SkipRegOp(Next_RegOp_out), .PHI0(apu_phi0_tocore), .DB_out(core_db_out),
    .Counter(core_counter), .PHI2(core_phi2), .RnW(core_rnw), .Addr(core_addr), .PHI1(core_phi1));  // open: SYNC
  Button Next_RegOp (.out(Next_RegOp_out));
  // Probe on core_counter
  AUXDumper dumper (.AUX({1'b0, apu_aux_b, apu_aux_a}), .PHI1(core_phi1), .Data(dumper_data), .Addr(dumper_addr));
  Hex_Digit_Display hex_digit_display_1 (.value(transp_latch_q_3));  // open: dp
  Register #(.trigger("high"), .width(16)) transp_latch (
    .D(core_addr), .en(core_addr[14]), .Q({transp_latch_q_3, transp_latch_q_2, transp_latch_q}),
    .clk(core_phi2));  // open: clr
  RAM #(.addrWidth(24), .dataWidth(32), .trigger("high")) aux_dump (
    .addr(dumper_addr), .we(1'b1), .oe(1'b0), .din(dumper_data), .dout(aux_dump_dout));
  Hex_Digit_Display hex_digit_display_2 (.value(transp_latch_q_2));  // open: dp
  Hex_Digit_Display hex_digit_display_3 (.value(transp_latch_q[7:4]));  // open: dp
  Hex_Digit_Display hex_digit_display_4 (.value(transp_latch_q[3:0]));  // open: dp
  // NoConnect on aux_dump_dout

  // Notes on the sheet:
  //   Load regdump here
  //   Last APU Register
  //   Taram-param-pam. Pam! Peep, peep, peep. Pipipipip, pip, pibibip
endmodule

module AUXDumper (
  input  PHI1,
  input  [23:0] AUX,
  output [23:0] Addr,
  output [31:0] Data
);

  wire and_1_out, counter_1_carry, counter_2_q, counter_3_q, s_r_ff_1_q;
  wire [31:0] aux_a_1_a, aux_b_1_a, fpadder_1_out, fpmultiplier_1_out;

  AUX_A aux_a_1 (.d(AUX[7:0]), .a(aux_a_1_a));
  AUX_B aux_b_1 (.d(AUX[23:8]), .a(aux_b_1_a));
  and and_1 (and_1_out, PHI1, ~s_r_ff_1_q);  // AND_Gate
  Counter #(.max('h7fffff), .ongoal("stay"), .width(23)) counter_1 (
    .Q(Addr[23:1]), .carry(counter_1_carry), .clk(and_1_out));  // open: load, D, count, up, clr
  FPMultiplier fpmultiplier_1 (.a(aux_a_1_a), .b(32'h3ecccccd), .out(fpmultiplier_1_out));
  Counter #(.max('h1), .width(1)) counter_2 (.Q(counter_2_q), .clk(and_1_out));  // open: load, D, count, carry, up, clr
  Counter #(.max('h1), .trigger("falling"), .width(1)) counter_3 (
    .Q(counter_3_q), .clk(and_1_out));  // open: load, D, count, carry, up, clr
  FPAdder fpadder_1 (.a(fpmultiplier_1_out), .b(aux_b_1_a), .out(fpadder_1_out));
  xnor xnor_1 (Addr[0], counter_2_q, counter_3_q);
  FPDivider fpdivider_1 (.a(fpadder_1_out), .b(32'h40000000), .out(Data));
  S_R_Flip_Flop s_r_ff_1 (.S(counter_1_carry), .Q(s_r_ff_1_q));  // open: clk, R, Qn, preset, reset

  // Notes on the sheet:
  //   * 0.4
  //   float->uint32_t Convert: https://gregstoll.com/~gregstoll/floattohex/
  //   a + b
  //   The invention of the org to make the ADDR tick EVERY half cycle.
  //    : 2
  //   normalized samples in range [0.0f; 1.0f]
endmodule

module AUX_A (
  input  [7:0] d,
  output [31:0] a
);

  ROM #(.dataWidth(32)) rom_1 (.addr(d), .data(a));

  // Notes on the sheet:
  //   0...255
  //   contents of rom_1 (hex, n*v repeats v):
  //   3ab77b8e 3d12a8ec 3d924925 3ddadec7 3e118b0c 3e3577e6 3e59364e 3e7cc69c 3e901495 3ea1af28 3eb33333
  //   3ec4a0e1 3ed5f85c 3ee739ce 3ef86563 3f04bda1 3d12a8ec 3d924925 3ddadec7 3e118b0c 3e3577e6 3e59364e
  //   3e7cc69c 3e901495 3ea1af28 3eb33333 3ec4a0e1 3ed5f85c 3ee739ce 3ef86563 3f04bda1 3f0d3dcb 3d924925
  //   3ddadec7 3e118b0c 3e3577e6 3e59364e 3e7cc69c 3e901495 3ea1af28 3eb33333 3ec4a0e1 3ed5f85c 3ee739ce
  //   3ef86563 3f04bda1 3f0d3dcb 3f15b343 3ddadec7 3e118b0c 3e3577e6 3e59364e 3e7cc69c 3e901495 3ea1af28
  //   3eb33333 3ec4a0e1 3ed5f85c 3ee739ce 3ef86563 3f04bda1 3f0d3dcb 3f15b343 3f1e1e1e 3e118b0c 3e3577e6
  //   3e59364e 3e7cc69c 3e901495 3ea1af28 3eb33333 3ec4a0e1 3ed5f85c 3ee739ce 3ef86563 3f04bda1 3f0d3dcb
  //   3f15b343 3f1e1e1e 3f267e6f 3e3577e6 3e59364e 3e7cc69c 3e901495 3ea1af28 3eb33333 3ec4a0e1 3ed5f85c
  //   3ee739ce 3ef86563 3f04bda1 3f0d3dcb 3f15b343 3f1e1e1e 3f267e6f 3f2ed44b 3e59364e 3e7cc69c 3e901495
  //   3ea1af28 3eb33333 3ec4a0e1 3ed5f85c 3ee739ce 3ef86563 3f04bda1 3f0d3dcb 3f15b343 3f1e1e1e 3f267e6f
  //   3f2ed44b 3f371fc4 3e7cc69c 3e901495 3ea1af28 3eb33333 3ec4a0e1 3ed5f85c 3ee739ce 3ef86563 3f04bda1
  //   3f0d3dcb 3f15b343 3f1e1e1e 3f267e6f 3f2ed44b 3f371fc4 3f3f60ef 3e901495 3ea1af28 3eb33333 3ec4a0e1
  //   3ed5f85c 3ee739ce 3ef86563 3f04bda1 3f0d3dcb 3f15b343 3f1e1e1e 3f267e6f 3f2ed44b 3f371fc4 3f3f60ef
  //   3f4797dd 3ea1af28 3eb33333 3ec4a0e1 3ed5f85c 3ee739ce 3ef86563 3f04bda1 3f0d3dcb 3f15b343 3f1e1e1e
  //   3f267e6f 3f2ed44b 3f371fc4 3f3f60ef 3f4797dd 3f4fc4a3 3eb33333 3ec4a0e1 3ed5f85c 3ee739ce 3ef86563
  //   3f04bda1 3f0d3dcb 3f15b343 3f1e1e1e 3f267e6f 3f2ed44b 3f371fc4 3f3f60ef 3f4797dd 3f4fc4a3 3f57e753
  //   3ec4a0e1 3ed5f85c 3ee739ce 3ef86563 3f04bda1 3f0d3dcb 3f15b343 3f1e1e1e 3f267e6f 3f2ed44b 3f371fc4
  //   3f3f60ef 3f4797dd 3f4fc4a3 3f57e753 3f600000 3ed5f85c 3ee739ce 3ef86563 3f04bda1 3f0d3dcb 3f15b343
  //   3f1e1e1e 3f267e6f 3f2ed44b 3f371fc4 3f3f60ef 3f4797dd 3f4fc4a3 3f57e753 3f600000 3f680ebc 3ee739ce
  //   3ef86563 3f04bda1 3f0d3dcb 3f15b343 3f1e1e1e 3f267e6f 3f2ed44b 3f371fc4 3f3f60ef 3f4797dd 3f4fc4a3
  //   3f57e753 3f600000 3f680ebc 3f701399 3ef86563 3f04bda1 3f0d3dcb 3f15b343 3f1e1e1e 3f267e6f 3f2ed44b
  //   3f371fc4 3f3f60ef 3f4797dd 3f4fc4a3 3f57e753 3f600000 3f680ebc 3f701399 3f780eaa 3f04bda1 3f0d3dcb
  //   3f15b343 3f1e1e1e 3f267e6f 3f2ed44b 3f371fc4 3f3f60ef 3f4797dd 3f4fc4a3 3f57e753 3f600000 3f680ebc
  //   3f701399 3f780eaa 3f800000
endmodule

module AUX_B (
  input  [15:0] d,
  output [31:0] a
);

  ROM #(.addrWidth(15), .dataWidth(32)) rom_1 (.addr(d[14:0]), .data(a));

  // Notes on the sheet:
  //   0...32767
  //   contents of rom_1 (hex, n*v repeats v):
  //   39f0dbd4 3cc007b4 3d3f0e2a 3d8e915b 3dbd229a 3deb3ca3 3e0c709f 3e230913 3e39688b 3e4f8fdb 3e657fd7
  //   3e7b394d 3e885e84 3e9305e6 3e9d932f 3ea806be 3c40856f 3d0fa7f6 3d6e36ed 3da5e8fe 3dd43e69 3e010ec1
  //   3e17c406 3e2e3fe1 3e44832b 3e5a8eb7 3e706356 3e8300eb 3e8db57e 3e984fc8 3ea2d028 3ead36fd 3cc007b4
  //   3d3f0e2a 3d8e915b 3dbd229a 3deb3ca3 3e0c709f 3e230913 3e39688b 3e4f8fdb 3e657fd7 3e7b394d 3e885e84
  //   3e9305e6 3e9d932f 3ea806be 3eb260f0 3d0fa7f6 3d6e36ed 3da5e8fe 3dd43e69 3e010ec1 3e17c406 3e2e3fe1
  //   3e44832b 3e5a8eb7 3e706356 3e8300eb 3e8db57e 3e984fc8 3ea2d028 3ead36fd 3eb784a4 3d3f0e2a 3d8e915b
  //   3dbd229a 3deb3ca3 3e0c709f 3e230913 3e39688b 3e4f8fdb 3e657fd7 3e7b394d 3e885e84 3e9305e6 3e9d932f
  //   3ea806be 3eb260f0 3ebca222 3d6e36ed 3da5e8fe 3dd43e69 3e010ec1 3e17c406 3e2e3fe1 3e44832b 3e5a8eb7
  //   3e706356 3e8300eb 3e8db57e 3e984fc8 3ea2d028 3ead36fd 3eb784a4 3ec1b977 3d8e915b 3dbd229a 3deb3ca3
  //   3e0c709f 3e230913 3e39688b 3e4f8fdb 3e657fd7 3e7b394d 3e885e84 3e9305e6 3e9d932f 3ea806be 3eb260f0
  //   3ebca222 3ec6caae 3da5e8fe 3dd43e69 3e010ec1 3e17c406 3e2e3fe1 3e44832b 3e5a8eb7 3e706356 3e8300eb
  //   3e8db57e 3e984fc8 3ea2d028 3ead36fd 3eb784a4 3ec1b977 3ecbd5d1 3dbd229a 3deb3ca3 3e0c709f 3e230913
  //   3e39688b 3e4f8fdb 3e657fd7 3e7b394d 3e885e84 3e9305e6 3e9d932f 3ea806be 3eb260f0 3ebca222 3ec6caae
  //   3ed0daec 3dd43e69 3e010ec1 3e17c406 3e2e3fe1 3e44832b 3e5a8eb7 3e706356 3e8300eb 3e8db57e 3e984fc8
  //   3ea2d028 3ead36fd 3eb784a4 3ec1b977 3ecbd5d1 3ed5da09 3deb3ca3 3e0c709f 3e230913 3e39688b 3e4f8fdb
  //   3e657fd7 3e7b394d 3e885e84 3e9305e6 3e9d932f 3ea806be 3eb260f0 3ebca222 3ec6caae 3ed0daec 3edad333
  //   3e010ec1 3e17c406 3e2e3fe1 3e44832b 3e5a8eb7 3e706356 3e8300eb 3e8db57e 3e984fc8 3ea2d028 3ead36fd
  //   3eb784a4 3ec1b977 3ecbd5d1 3ed5da09 3edfc674 3e0c709f 3e230913 3e39688b 3e4f8fdb 3e657fd7 3e7b394d
  //   3e885e84 3e9305e6 3e9d932f 3ea806be 3eb260f0 3ebca222 3ec6caae 3ed0daec 3edad333 3ee4b3d8 3e17c406
  //   3e2e3fe1 3e44832b 3e5a8eb7 3e706356 3e8300eb 3e8db57e 3e984fc8 3ea2d028 3ead36fd 3eb784a4 3ec1b977
  //   3ecbd5d1 3ed5da09 3edfc674 3ee99b68 3e230913 3e39688b 3e4f8fdb 3e657fd7 3e7b394d 3e885e84 3e9305e6
  //   3e9d932f 3ea806be 3eb260f0 3ebca222 3ec6caae 3ed0daec 3edad333 3ee4b3d8 3eee7d2e 3e2e3fe1 3e44832b
  //   3e5a8eb7 3e706356 3e8300eb 3e8db57e 3e984fc8 3ea2d028 3ead36fd 3eb784a4 3ec1b977 3ecbd5d1 3ed5da09
  //   3edfc674 3ee99b68 3ef35936 3bc0c48a 3cefbb5a 3d56aa32 3d9a40f1 3dc8b438 3df6b0bb 3e121c1f 3e28a641
  //   3e3ef79a 3e551102 3e6af34a 3e804f9f 3e8b0ad4 3e95aba7 3ea03278 3eaa9fa7 3c9034de 3d2762c6 3d82da35
  //   3db1898a 3ddfc135 3e06c180 3e1d6856 3e33d5f9 3e4a0b3f 3e6008fd 3e75d001 3e85b08c 3e905e84 3e9af24a
  //   3ea56c3e 3eafccbf 3cefbb5a 3d56aa32 3d9a40f1 3dc8b438 3df6b0bb 3e121c1f 3e28a641 3e3ef79a 3e551102
  //   3e6af34a 3e804f9f 3e8b0ad4 3e95aba7 3ea03278 3eaa9fa7 3eb4f391 3d2762c6 3d82da35 3db1898a 3ddfc135
  //   3e06c180 3e1d6856 3e33d5f9 3e4a0b3f 3e6008fd 3e75d001 3e85b08c 3e905e84 3e9af24a 3ea56c3e 3eafccbf
  //   3eba1429 3d56aa32 3d9a40f1 3dc8b438 3df6b0bb 3e121c1f 3e28a641 3e3ef79a 3e551102 3e6af34a 3e804f9f
  //   3e8b0ad4 3e95aba7 3ea03278 3eaa9fa7 3eb4f391 3ebf2e91 3d82da35 3db1898a 3ddfc135 3e06c180 3e1d6856
  //   3e33d5f9 3e4a0b3f 3e6008fd 3e75d001 3e85b08c 3e905e84 3e9af24a 3ea56c3e 3eafccbf 3eba1429 3ec442d6
  //   3d9a40f1 3dc8b438 3df6b0bb 3e121c1f 3e28a641 3e3ef79a 3e551102 3e6af34a 3e804f9f 3e8b0ad4 3e95aba7
  //   3ea03278 3eaa9fa7 3eb4f391 3ebf2e91 3ec95101 3db1898a 3ddfc135 3e06c180 3e1d6856 3e33d5f9 3e4a0b3f
  //   3e6008fd 3e75d001 3e85b08c 3e905e84 3e9af24a 3ea56c3e 3eafccbf 3eba1429 3ec442d6 3ece591f 3dc8b438
  //   3df6b0bb 3e121c1f 3e28a641 3e3ef79a 3e551102 3e6af34a 3e804f9f 3e8b0ad4 3e95aba7 3ea03278 3eaa9fa7
  //   3eb4f391 3ebf2e91 3ec95101 3ed35b39 3ddfc135 3e06c180 3e1d6856 3e33d5f9 3e4a0b3f 3e6008fd 3e75d001
  //   3e85b08c 3e905e84 3e9af24a 3ea56c3e 3eafccbf 3eba1429 3ec442d6 3ece591f 3ed8575b 3df6b0bb 3e121c1f
  //   3e28a641 3e3ef79a 3e551102 3e6af34a 3e804f9f 3e8b0ad4 3e95aba7 3ea03278 3eaa9fa7 3eb4f391 3ebf2e91
  //   3ec95101 3ed35b39 3edd4d90 3e06c180 3e1d6856 3e33d5f9 3e4a0b3f 3e6008fd 3e75d001 3e85b08c 3e905e84
  //   3e9af24a 3ea56c3e 3eafccbf 3eba1429 3ec4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
endmodule

module Fake6502 (
  input  PHI0,
  input  RDY,
  input  SO,
  input  n_NMI,
  input  n_IRQ,
  input  n_RES,
  input  [7:0] DB_in,
  input  SkipRegOp,
  output PHI1,
  output PHI2,
  output RnW,
  output SYNC,
  output [15:0] Addr,
  output [7:0] DB_out,
  output [31:0] Counter
);

  wire [23:0] redump_redump_addr;
  wire [31:0] regdump_data;

  ROM #(.addrWidth(24), .dataWidth(32)) regdump (.addr(redump_redump_addr), .data(regdump_data));
  RegDumpProcessor redump (
    .SkipRegOp(SkipRegOp), .PHI0(PHI0), .regdump_data(regdump_data), .Core_AB(Addr), .Core_DB(DB_out),
    .redump_addr(redump_redump_addr), .Core_RnW(RnW), .PhiDecCnt(Counter));
  not not_1 (PHI1, PHI0);

  assign PHI2 = PHI0;
  assign SYNC = 1'b0;

  // Notes on the sheet:
  //   N.C.
  //   contents of regdump (hex, n*v repeats v):
  //   2 10 6 1f15 9 c017 98 1f15 6 10 a0d 1000 4 1004 4 100c 6 8 6 f15 2 214 2f1 116 6 16 1b3 116 6 16 210
  //   1000 4 1004 4 100c 6 8 6 f15 100 1000 c 1004 c 8 c 100c 2 214 4f6 116 6 16 1b3 116 6 16 297 1000 c
  //   1004 c 8 c 100c 2 214 4f6 116 6 16 1b3 116 6 16 297 1000 c 1004 c 8 c 100c 2 214 4f5 116 6 16 1b3
  //   116 6 16 297 1000 c 1004 c 8 c 100c 2 214 4f6 116 6 16 1b3 116 6 16 297 1000 c 1004 c 8 c 100c 2 214
  //   4f6 116 6 16 1b3 116 6 16 297 1000 c 1004 c 8 c 100c 2 214 2f0 116 6 16 1b3 116 6 16 297 1000 c 1004
  //   c 8 c 100c 2 1000 4 1004 4 100c 6 8 6 f15 100 1000 c 1004 c 8 c 100c 2 1000 4 1004 4 100c 6 8 6 f15
  //   4c1 800c 8 80d 15 80f 8 2 174 ff08 8 809 15 80b 8 c90a 101 1004 8 805 15 807 8 6 101 1000 8 801 ec
  //   8d10 b 1011 b 4012 b a913 b f15 7 f15 6a1e 214 2f0 116 6 16 1b3 116 6 16 359 800c 8 80d 15 80f 8 e
  //   132 ff08 8 809 15 80b 8 d50a af 1004 8 805 b7 1000 8 801 695b 214 4f6 116 6 16 1b3 116 6 16 2f9 800c
  //   8 80d 13a ff08 8 809 15 80b 8 c90a af 1004 8 805 b7 1000 8 801 67ca 214 4f5 116 6 16 1b3 116 6 16
  //   359 800c 8 80d 15 80f 8 790e 163 ff08 8 809 15 80b 8 c90a af 1004 8 805 b7 1000 8 801 6725 214 4f6
  //   116 6 16 1b3 116 6 16 359 800c 8 80d 15 80f 8 e 132 ff08 8 809 15 80b 8 d50a af 1004 8 805 b7 1000 8
  //   801 6756 214 4f6 116 6 16 1b3 116 6 16 2f9 800c 8 80d 13a ff08 8 809 15 80b 8 c90a af 1004 8 805 b7
  //   1000 8 801 67c7 214 4f6 116 6 16 1b3 116 6 16 2f9 800c 8 80d 13a ff08 8 809 15 80b 8 be0a af 1004 8
  //   805 b7 1000 8 801 67ca 214 4f5 116 6 16 1b3 116 6 16 359 800c 8 80d 15 80f 8 790e 1ca ff08 8 809 15
  //   80b 8 c90a af 1004 8 805 b7 1000 8 801 66bd 214 4f5 116 6 16 1b3 116 6 16 359 800c 8 80d 15 80f 8 e
  //   132 ff08 8 809 15 80b 8 d50a af 1004 8 805 b7 1000 8 801 6758 214 4f6 116 6 16 1b3 116 6 16 328 800c
  //   8 80d 13a ff08 8 809 15 80b 8 c90a af 1004 8 805 b7 1000 8 801 6797 214 4f5 116 6 16 1b3 116 6 16
  //   359 800c 8 80d 15 80f 8 790e 179 ff08 8 809 15 80b 8 c90a af 1004 8 805 b7 1000 8 801 6711 214 4f6
  //   116 6 16 1b3 116 6 16 359 800c 8 80d 15 80f 8 e 132 ff08 8 809 15 80b 8 d50a af 1004 8 805 b7 1000 8
  //   801 6752 214 4f6 116 6 16 1b3 116 6 16 340 800c 8 80d 13a ff08 8 809 15 80b 8 e20a af 1004 8 805 b7
  //   1000 8 801 6785 214 4f5 116 6 16 1b3 116 6 16 2f9 800c 8 80d 13a ff08 8 809 15 80b 8 f00a af 1004 8
  //   805 b7 1000 8 801 67c9 214 4f6 116 6 16 1b3 116 6 16 2f9 800c 8 80d 10a 8 8 809 b7 1004 8 805 b7
  //   1000 8 801 680f 214 4f5 116 6 16 1b3 116 6 16 359 800c 8 80d 15 80f 8 790e 1c3 ff08 8 809 15 80b 8
  //   c90a af 1004 8 805 b7 1000 8 801 66c5 214 4f6 116 6 16 1b3 116 6 16 359 800c 8 80d 15 80f 8 e 132
  //   ff08 8 809 15 80b 8 d50a af 1004 8 805 b7 1000 8 801 6754 214 4f6 116 6 16 1b3 116 6 16 33f 800c 8
  //   80d 13a ff08 8 809 15 80b 8 e20a af 1004 8 805 b7 1000 8 801 6783 214 4f6 116 6 16 1b3 116 6 16 2f9
  //   800c 8 80d 13a ff08 8 809 15 80b 8 f00a af 1004 8 805 b7 1000 8 801 67cb 214 4f6 116 6 16 1b3 116 6
  //   16 2f9 800c 8 80d 10a 8 8 809 b7 1004 8 805 b7 1000 8 801 680d 214 4f5 116 6 16 1b3 116 6 16 359
  //   800c 8 80d 15 80f 8 790e 179 ff08 8 809 15 90b 8 400a af 1004 8 805 b7 1000 8 801 670e 214 4f5 116 6
  //   16 1b3 116 6 16 359 800c 8 80d 15 80f 8 e 132 ff08 8 809 15 90b 8 530a af 1004 8 805 b7 1000 8 801
  //   6756 214 4f6 116 6 16 1b3 116 6 16 33f 800c 8 80d 13a ff08 8 809 15 90b 8 670a af 1004 8 805 b7 1000
  //   8 801 6786 214 4f5 116 6 16 1b3 116 6 16 2f9 800c 8 80d 13a ff08 8 809 15 90b 8 7d0a af 1004 8 805
  //   b7 1000 8 801 67c8 214 4f5 116 6 16 1b3 116 6 16 2f9 800c 8 80d 10a 8 8 809 b7 1004 8 805 b7 1000 8
  //   801 6810 214 4f6 116 6 16 1b3 116 6 16 359 800c 8 80d 15 80f 8 790e 1c3 ff08 8 809 15 90b 8 400a af
  //   1004 8 805 b7 1000 8 801 66c3 214 4f6 116 6 16 1b3 116 6 16 359 800c 8 80d 15 80f 8 e 132 ff08 8 809
  //   15 90b 8 530a af 1004 8 805 b7 1000 8 801 6756 214 4f6 116 6 16 1b3 116 6 16 33f 800c 8 80d 13a ff08
  //   8 809 15 90b 8 670a af 1004 8 805 b7 1000 8 801 6783 214 4f6 116 6 16 1b3 116 6 16 2f9 800c 8 80d
  //   13a ff08 8 809 15 90b 8 7d0a af 1004 8 805 b7 1000 8 801 67c8 214 4f5 116 6 16 1b3 116 6 16 2f9 800c
  //   8 80d 10a 8 8 809 b7 1004 8 805 b7 1000 8 801 6810 214 4f6 116 6 16 1b3 116 6 16 359 800c 8 80d 15
  //   80f 8 790e 1a8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
  //   N.C.
  //   N.C.
  //   Load regdump here
endmodule

module WRAM (
  input  M2,
  input  [15:0] Addr,
  input  [7:0] DB_in,
  input  RnW,
  input  n_RES,
  output [7:0] DB_out
);

  wire and_1_out, and_2_out, comparator_1_gt, nor_1_out, or_1_out;
  wire [7:0] cpumem_dout;

  nor nor_1 (nor_1_out, Addr[11], Addr[12], Addr[13], Addr[14], Addr[15]);
  Comparator #(.mode("unsigned"), .width(16)) comparator_1 (
    .a(Addr), .b(16'h8000), .gt(comparator_1_gt));  // open: eq, lt
  or or_1 (or_1_out, nor_1_out, comparator_1_gt);
  RAM #(.addrWidth(16)) cpumem (.addr(Addr), .we(and_1_out), .oe(and_2_out), .clk(M2), .din(DB_in), .dout(cpumem_dout));
  and and_1 (and_1_out, or_1_out, n_RES, ~RnW);  // AND_Gate
  and and_2 (and_2_out, or_1_out, n_RES, RnW);
  assign DB_out = n_RES ? cpumem_dout : 8'bz;  // Controlled_Buffer controlled_buffer_1

  // Notes on the sheet:
  //   Load 64K CPU Memory dump here (with DPCM samples)
endmodule

module RegDumpProcessor (
  input  PHI0,
  input  SkipRegOp,
  input  [31:0] regdump_data,
  output Core_RnW,
  output [15:0] Core_AB,
  output [7:0] Core_DB,
  output [23:0] redump_addr,
  output [31:0] PhiDecCnt
);

  wire and_1_out, and_2_out, cnt_ovf_reg_q, comparator_1_eq, comparator_1_gt, comparator_2_eq,
       comparator_3_gt, multiplexer_1_out, multiplexer_2_out, not_1_out, or_1_out, or_2_out, or_3_out;
  wire [7:0] undriven;
  wire [15:0] or_4_out;
  wire [31:0] delta_phi_word_q, multiplexer_3_out, multiplexer_4_out, regop_word_q, subtractor_1_out;

  or or_1 (or_1_out, SkipRegOp, cnt_ovf_reg_q);
  Comparator #(.mode("unsigned"), .width(32)) comparator_1 (
    .a(regdump_data), .b(32'h2), .gt(comparator_1_gt), .eq(comparator_1_eq));  // open: lt
  Subtractor #(.width(32)) subtractor_1 (.a(regdump_data), .b(32'h2), .out(subtractor_1_out));  // open: bin, bout
  Multiplexer multiplexer_1 (.in0(1'b0), .in1(1'b1), .out(multiplexer_1_out), .sel(or_1_out));
  Multiplexer multiplexer_2 (.in0(1'b1), .in1(1'b0), .out(multiplexer_2_out), .sel(or_1_out));
  Multiplexer #(.width(32)) multiplexer_3 (.in0(regdump_data), .in1(32'h20), .out(multiplexer_3_out), .sel(SkipRegOp));
  Register #(.width(32)) delta_phi_word (.D(regdump_data), .Q(delta_phi_word_q), .clk(cnt_ovf_reg_q));  // open: en, clr
  or or_2 (or_2_out, comparator_1_gt, comparator_1_eq);
  Counter #(.max('hffffffff), .ongoal("stay"), .width(32)) phi_dec_cnt (
    .load(multiplexer_1_out), .D(multiplexer_3_out), .count(multiplexer_2_out), .Q(PhiDecCnt), .up(1'b0),
    .clk(PHI0));  // open: carry, clr
  Register #(.width(32)) regop_word (
    .D(regdump_data), .Q(regop_word_q), .clk(and_1_out), .clr(cnt_ovf_reg_q));  // open: en
  Multiplexer #(.width(32)) multiplexer_4 (
    .in0(32'h1), .in1(subtractor_1_out), .out(multiplexer_4_out), .sel(or_2_out));
  Comparator #(.mode("unsigned"), .width(32)) comparator_2 (
    .a(PhiDecCnt), .b({32{1'b0}}), .eq(comparator_2_eq));  // open: gt, lt
  Comparator #(.mode("unsigned"), .width(32)) comparator_3 (
    .a(delta_phi_word_q), .b({32{1'b0}}), .gt(comparator_3_gt));  // open: eq, lt
  and and_1 (and_1_out, PHI0, comparator_3_gt, comparator_2_eq, ~cnt_ovf_reg_q);  // AND_Gate
  Register #(.width(1)) cnt_ovf_reg (.D(comparator_2_eq), .Q(cnt_ovf_reg_q), .clk(PHI0));  // open: en, clr
  or or_3 (or_3_out, and_1_out, cnt_ovf_reg_q);
  assign or_4_out = 16'h4000 | {{11{1'b0}}, regop_word_q[4:0]};  // OR_Gate or_4, 16 bits wide
  Multiplexer multiplexer_5 (.in0(1'b1), .in1(regop_word_q[7]), .out(Core_RnW), .sel(and_1_out));
  // NoConnect on undriven
  and and_2 (and_2_out, and_1_out, not_1_out);
  not not_1 (not_1_out, regop_word_q[7]);
  Multiplexer #(.width(16)) multiplexer_6 (.in0({16{1'b0}}), .in1(or_4_out), .out(Core_AB), .sel(and_1_out));
  Multiplexer #(.width(8)) multiplexer_7 (.in0(undriven), .in1(regop_word_q[15:8]), .out(Core_DB), .sel(and_2_out));
  Counter #(.max('hffffff), .ongoal("stay"), .trigger("falling"), .width(24)) addr_cnt (
    .load(1'b0), .count(1'b1), .Q(redump_addr), .up(1'b1), .clk(or_3_out));  // open: D, carry, clr

  // Notes on the sheet:
  //   Load/Decrement Setup (1: Load; 0: Decrement)
  //   Do RegOp
  //   Load PHI Counter
  //   RegOp Setup
  //   Reg Index (0-0x1f)
  //   Reg Address
  //   Value (if write)
  //   1: Read register
  //   https://github.com/emu-russia/breaknes/blob/main/BreaksAPU/NSFPlayerInterop/RegDumpProcessor.cpp
  //   1: RegOp + Write
  //   Falling edge
  //   Default: Read address 0x0000
endmodule
