// Logisim project APU_Evo.circ as structural Verilog: 99 circuits, main circuit APU
module APU (
  input  CLK,
  input  n_RES,
  input  n_IRQ,
  input  n_NMI,
  input  DBG,
  input  [7:0] D_In,
  output M2,
  output RnW,
  output n_IN0,
  output n_IN1,
  output OUT_0,
  output OUT_1,
  output OUT_2,
  output [15:0] Ax,
  output [7:0] D_Out,
  output [7:0] AUX_A,
  output [14:0] AUX_B
);

  wire clk_div_n_m2, clk_div_phi0, io_out_0, io_out_1, io_out_2, lock_apu_lock, m6502_phi1, m6502_phi2,
       m6502_rnw, m6502_sync, nor_1_out, nor_2_out, not_1_out, not_2_out, not_3_out, not_4_out, not_5_out,
       not_6_out, not_7_out, not_8_out, not_9_out, not_10_out, not_11_out, not_12_out, not_13_out,
       not_14_out, regs_predecode_n_regrd, regs_predecode_n_regwr, rw_decoder_rd, rw_decoder_wr,
       soft_clk_aclk, soft_clk_int, soft_clk_n_aclk, soft_clk_n_lfo1, soft_clk_n_lfo2, sound_gen_apu_rw,
       sound_gen_dmcint, sound_gen_rdy;
  wire [7:0] dbus_db_out, m6502_d_out;
  wire [15:0] m6502_ax, sound_gen_apu_ax;
  wire [28:0] regops_n_r4018;

  not not_1 (not_1_out, CLK);
  not not_2 (not_2_out, n_RES);
  not not_3 (not_3_out, n_IRQ);
  nor nor_1 (nor_1_out, not_3_out, soft_clk_int);
  DIV clk_div (.n_CLK(not_1_out), .PHI2(m6502_phi2), .PHI0(clk_div_phi0), .n_M2(clk_div_n_m2));
  RegPredecode regs_predecode (
    .CPU_Ax(m6502_ax), .CPU_RnW(m6502_rnw), .n_REGRD(regs_predecode_n_regrd), .n_REGWR(regs_predecode_n_regwr));
  not not_4 (not_4_out, not_2_out);
  RegSel regops (
    .PHI1(m6502_phi1), .DBG(DBG), .n_REGRD(regs_predecode_n_regrd), .n_REGWR(regs_predecode_n_regwr),
    .APU_Ax(sound_gen_apu_ax), .n_R4018(regops_n_r4018[0]), .n_R401A(regops_n_r4018[1]),
    .n_R4015(regops_n_r4018[2]), .W4002(regops_n_r4018[3]), .W4001(regops_n_r4018[4]),
    .W4005(regops_n_r4018[5]), .W4006(regops_n_r4018[6]), .W4008(regops_n_r4018[7]),
    .W400A(regops_n_r4018[8]), .W400B(regops_n_r4018[9]), .W400E(regops_n_r4018[10]),
    .W4013(regops_n_r4018[11]), .W4012(regops_n_r4018[12]), .W4010(regops_n_r4018[13]),
    .W4014(regops_n_r4018[14]), .n_R4019(regops_n_r4018[15]), .W401A(regops_n_r4018[16]),
    .W4003(regops_n_r4018[17]), .W4007(regops_n_r4018[18]), .W4004(regops_n_r4018[19]),
    .W400C(regops_n_r4018[20]), .W4000(regops_n_r4018[21]), .W4015(regops_n_r4018[22]),
    .W4011(regops_n_r4018[23]), .W400F(regops_n_r4018[24]), .n_R4017(regops_n_r4018[25]),
    .n_R4016(regops_n_r4018[26]), .W4016(regops_n_r4018[27]), .W4017(regops_n_r4018[28]));
  Core m6502 (
    .PHI0(clk_div_phi0), .n_NMI(n_NMI), .n_IRQ(nor_1_out), .n_RES(not_4_out), .RDY(sound_gen_rdy),
    .D_in(dbus_db_out), .PHI1(m6502_phi1), .PHI2(m6502_phi2), .RnW(m6502_rnw), .SYNC(m6502_sync),
    .Ax(m6502_ax), .D_Out(m6502_d_out));
  // NoConnect on m6502_sync
  SoftCLK soft_clk (
    .PHI1(m6502_phi1), .PHI2(m6502_phi2), .RES(not_2_out), .DMCINT(sound_gen_dmcint),
    .n_R4015(regops_n_r4018[2]), .W4017(regops_n_r4018[28]), .D_In(dbus_db_out), .ACLK(soft_clk_aclk),
    .n_ACLK(soft_clk_n_aclk), .n_LFO1(soft_clk_n_lfo1), .n_LFO2(soft_clk_n_lfo2), .INT(soft_clk_int),
    .D_Out(m6502_d_out));
  SoundGenerators sound_gen (
    .PHI1(m6502_phi1), .PHI2(m6502_phi2), .ACLK(soft_clk_aclk), .n_ACLK(soft_clk_n_aclk),
    .n_LFO1(soft_clk_n_lfo1), .n_LFO2(soft_clk_n_lfo2), .RES(not_2_out), .RegOps(regops_n_r4018),
    .D_In(dbus_db_out), .CPU_Ax(m6502_ax), .CPU_RnW(m6502_rnw), .LOCK(lock_apu_lock),
    .DMCINT(sound_gen_dmcint), .RDY(sound_gen_rdy), .APU_RW(sound_gen_apu_rw), .APU_Ax(sound_gen_apu_ax),
    .D_Out(m6502_d_out), .AUX_A(AUX_A), .AUX_B(AUX_B));
  not not_5 (not_5_out, not_2_out);
  nor nor_2 (nor_2_out, not_5_out, DBG);
  OUT_Ports io (
    .W4016(regops_n_r4018[27]), .ACLK(soft_clk_aclk), .n_ACLK(soft_clk_n_aclk), .D_In(dbus_db_out),
    .OUT_0(io_out_0), .OUT_1(io_out_1), .OUT_2(io_out_2));
  DebugLock lock (
    .W401A(regops_n_r4018[16]), .n_ACLK(soft_clk_n_aclk), .RES(not_2_out), .D_In(dbus_db_out),
    .APU_LOCK(lock_apu_lock));
  RWDecode rw_decoder (
    .APU_RW(sound_gen_apu_rw), .n_R4015(regops_n_r4018[2]), .DBG(DBG), .n_REGRD(regs_predecode_n_regrd),
    .WR(rw_decoder_wr), .RD(rw_decoder_rd));
  not not_6 (not_6_out, nor_2_out);
  not not_7 (not_7_out, clk_div_n_m2);
  assign M2 = not_6_out ? not_7_out : 1'bz;  // Controlled_Buffer controlled_buffer_1
  not not_8 (not_8_out, not_2_out);
  assign RnW = not_8_out ? sound_gen_apu_rw : 1'bz;  // Controlled_Buffer controlled_buffer_2
  not not_9 (not_9_out, not_2_out);
  assign n_IN0 = not_9_out ? regops_n_r4018[26] : 1'bz;  // Controlled_Buffer controlled_buffer_3
  not not_10 (not_10_out, not_2_out);
  assign n_IN1 = not_10_out ? regops_n_r4018[25] : 1'bz;  // Controlled_Buffer controlled_buffer_4
  not not_11 (not_11_out, not_2_out);
  assign OUT_0 = not_11_out ? io_out_0 : 1'bz;  // Controlled_Buffer controlled_buffer_5
  not not_12 (not_12_out, not_2_out);
  assign OUT_1 = not_12_out ? io_out_1 : 1'bz;  // Controlled_Buffer controlled_buffer_6
  not not_13 (not_13_out, not_2_out);
  assign OUT_2 = not_13_out ? io_out_2 : 1'bz;  // Controlled_Buffer controlled_buffer_7
  not not_14 (not_14_out, not_2_out);
  assign Ax = not_14_out ? sound_gen_apu_ax : 16'bz;  // Controlled_Buffer controlled_buffer_8
  DataBusPads dbus (
    .Pads_In(D_In), .DB_In(m6502_d_out), .RD(rw_decoder_rd), .WR(rw_decoder_wr), .DB_Out(dbus_db_out),
    .Pads_Out(D_Out));

  // Notes on the sheet:
  //   RES
  //   NotDBG_RES
endmodule

module APU_NoCore (
  input  CLK,
  input  n_RES,
  input  n_IRQ,
  input  PHI1_FromCore,
  input  PHI2_FromCore,
  input  [15:0] Addr_FromCore,
  input  [7:0] DB_FromCore,
  input  RnW_FromCore,
  input  DBG,
  input  [7:0] D_In,
  output PHI0_ToCore,
  output M2,
  output RnW,
  output n_IN0,
  output n_IN1,
  output OUT_0,
  output OUT_1,
  output OUT_2,
  output RDY_ToCore,
  output n_IRQ_ToCore,
  output [15:0] Ax,
  output [7:0] DB_ToCore,
  output [7:0] D_Out,
  output [7:0] AUX_A,
  output [14:0] AUX_B
);

  wire clk_div_n_m2, io_out_0, io_out_1, io_out_2, lock_apu_lock, nor_2_out, not_1_out, not_2_out, not_3_out,
       not_4_out, not_5_out, not_6_out, not_7_out, not_8_out, not_9_out, not_10_out, not_11_out, not_12_out,
       not_13_out, regs_predecode_n_regrd, regs_predecode_n_regwr, rw_decoder_rd, rw_decoder_wr,
       soft_clk_aclk, soft_clk_int, soft_clk_n_aclk, soft_clk_n_lfo1, soft_clk_n_lfo2, sound_gen_apu_rw,
       sound_gen_dmcint;
  wire [15:0] sound_gen_apu_ax;
  wire [28:0] regops_n_r4018;

  not not_1 (not_1_out, CLK);
  not not_2 (not_2_out, n_RES);
  not not_3 (not_3_out, n_IRQ);
  DIV clk_div (.n_CLK(not_1_out), .PHI2(PHI2_FromCore), .PHI0(PHI0_ToCore), .n_M2(clk_div_n_m2));
  nor nor_1 (n_IRQ_ToCore, not_3_out, soft_clk_int);
  RegPredecode regs_predecode (
    .CPU_Ax(Addr_FromCore), .CPU_RnW(RnW_FromCore), .n_REGRD(regs_predecode_n_regrd),
    .n_REGWR(regs_predecode_n_regwr));
  RegSel regops (
    .PHI1(PHI1_FromCore), .DBG(DBG), .n_REGRD(regs_predecode_n_regrd), .n_REGWR(regs_predecode_n_regwr),
    .APU_Ax(sound_gen_apu_ax), .n_R4018(regops_n_r4018[0]), .n_R401A(regops_n_r4018[1]),
    .n_R4015(regops_n_r4018[2]), .W4002(regops_n_r4018[3]), .W4001(regops_n_r4018[4]),
    .W4005(regops_n_r4018[5]), .W4006(regops_n_r4018[6]), .W4008(regops_n_r4018[7]),
    .W400A(regops_n_r4018[8]), .W400B(regops_n_r4018[9]), .W400E(regops_n_r4018[10]),
    .W4013(regops_n_r4018[11]), .W4012(regops_n_r4018[12]), .W4010(regops_n_r4018[13]),
    .W4014(regops_n_r4018[14]), .n_R4019(regops_n_r4018[15]), .W401A(regops_n_r4018[16]),
    .W4003(regops_n_r4018[17]), .W4007(regops_n_r4018[18]), .W4004(regops_n_r4018[19]),
    .W400C(regops_n_r4018[20]), .W4000(regops_n_r4018[21]), .W4015(regops_n_r4018[22]),
    .W4011(regops_n_r4018[23]), .W400F(regops_n_r4018[24]), .n_R4017(regops_n_r4018[25]),
    .n_R4016(regops_n_r4018[26]), .W4016(regops_n_r4018[27]), .W4017(regops_n_r4018[28]));
  SoftCLK soft_clk (
    .PHI1(PHI1_FromCore), .PHI2(PHI2_FromCore), .RES(not_2_out), .DMCINT(sound_gen_dmcint),
    .n_R4015(regops_n_r4018[2]), .W4017(regops_n_r4018[28]), .D_In(DB_ToCore), .ACLK(soft_clk_aclk),
    .n_ACLK(soft_clk_n_aclk), .n_LFO1(soft_clk_n_lfo1), .n_LFO2(soft_clk_n_lfo2), .INT(soft_clk_int),
    .D_Out(DB_FromCore));
  SoundGenerators sound_gen (
    .PHI1(PHI1_FromCore), .PHI2(PHI2_FromCore), .ACLK(soft_clk_aclk), .n_ACLK(soft_clk_n_aclk),
    .n_LFO1(soft_clk_n_lfo1), .n_LFO2(soft_clk_n_lfo2), .RES(not_2_out), .RegOps(regops_n_r4018),
    .D_In(DB_ToCore), .CPU_Ax(Addr_FromCore), .CPU_RnW(RnW_FromCore), .LOCK(lock_apu_lock),
    .DMCINT(sound_gen_dmcint), .RDY(RDY_ToCore), .APU_RW(sound_gen_apu_rw), .APU_Ax(sound_gen_apu_ax),
    .D_Out(DB_FromCore), .AUX_A(AUX_A), .AUX_B(AUX_B));
  not not_4 (not_4_out, not_2_out);
  nor nor_2 (nor_2_out, not_4_out, DBG);
  OUT_Ports io (
    .W4016(regops_n_r4018[27]), .ACLK(soft_clk_aclk), .n_ACLK(soft_clk_n_aclk), .D_In(DB_ToCore),
    .OUT_0(io_out_0), .OUT_1(io_out_1), .OUT_2(io_out_2));
  DebugLock lock (
    .W401A(regops_n_r4018[16]), .n_ACLK(soft_clk_n_aclk), .RES(not_2_out), .D_In(DB_ToCore),
    .APU_LOCK(lock_apu_lock));
  RWDecode rw_decoder (
    .APU_RW(sound_gen_apu_rw), .n_R4015(regops_n_r4018[2]), .DBG(DBG), .n_REGRD(regs_predecode_n_regrd),
    .WR(rw_decoder_wr), .RD(rw_decoder_rd));
  not not_5 (not_5_out, clk_div_n_m2);
  not not_6 (not_6_out, nor_2_out);
  assign M2 = not_6_out ? not_5_out : 1'bz;  // Controlled_Buffer controlled_buffer_1
  not not_7 (not_7_out, not_2_out);
  assign RnW = not_7_out ? sound_gen_apu_rw : 1'bz;  // Controlled_Buffer controlled_buffer_2
  not not_8 (not_8_out, not_2_out);
  assign n_IN0 = not_8_out ? regops_n_r4018[26] : 1'bz;  // Controlled_Buffer controlled_buffer_3
  not not_9 (not_9_out, not_2_out);
  assign n_IN1 = not_9_out ? regops_n_r4018[25] : 1'bz;  // Controlled_Buffer controlled_buffer_4
  not not_10 (not_10_out, not_2_out);
  assign OUT_0 = not_10_out ? io_out_0 : 1'bz;  // Controlled_Buffer controlled_buffer_5
  not not_11 (not_11_out, not_2_out);
  assign OUT_1 = not_11_out ? io_out_1 : 1'bz;  // Controlled_Buffer controlled_buffer_6
  not not_12 (not_12_out, not_2_out);
  assign OUT_2 = not_12_out ? io_out_2 : 1'bz;  // Controlled_Buffer controlled_buffer_7
  not not_13 (not_13_out, not_2_out);
  assign Ax = not_13_out ? sound_gen_apu_ax : 16'bz;  // Controlled_Buffer controlled_buffer_8
  DataBusPads dbus (
    .Pads_In(D_In), .DB_In(DB_FromCore), .RD(rw_decoder_rd), .WR(rw_decoder_wr), .DB_Out(DB_ToCore),
    .Pads_Out(D_Out));

  // Notes on the sheet:
  //   RES
  //   NotDBG_RES
endmodule

module DMC (
  input  ACLK,
  input  n_ACLK,
  input  PHI1,
  input  RES,
  input  RnW,
  input  LOCK,
  input  W4010,
  input  W4011,
  input  W4012,
  input  W4013,
  input  W4015,
  input  n_R4015,
  input  [7:0] Dx_In,
  output n_DMCAB,
  output RUNDMC,
  output DMCRDY,
  output DMCINT,
  output [7:0] Dx_Out,
  output [6:0] DMC_Out,
  output [15:0] DMC_Addr
);

  wire ctrl_reg_loopmode, ctrl_reg_n_irqen, dpcm_ctrl_dstep, dpcm_ctrl_nstep, dpcm_ctrl_pcm, dpcm_out_dout,
       sbuf_n_bout;
  wire [1:0] dpcm_ctrl_bload, dpcm_ctrl_dsload;
  wire [2:0] sbcnt_n_nout;
  wire [3:0] ctrl_reg_f_out;
  wire [7:0] addr_reg_addr_out, scnt_in_cnt_out;
  wire [8:0] decoder_fr_out;

  DPCM_AddressReg addr_reg (.n_ACLK(n_ACLK), .W4012(W4012), .Dx_In(Dx_In), .Addr_Out(addr_reg_addr_out));
  DPCM_Control dpcm_ctrl (
    .ACLK(ACLK), .n_ACLK(n_ACLK), .PHI1(PHI1), .RES(RES), .RnW(RnW), .LOCK(LOCK), .W4015(W4015),
    .n_R4015(n_R4015), .LOOPMod(ctrl_reg_loopmode), .n_IRQEN(ctrl_reg_n_irqen), .DOUT(dpcm_out_dout),
    .n_NOUT(sbcnt_n_nout[0]), .SOUT(sbcnt_n_nout[1]), .DFLOAD(sbcnt_n_nout[2]), .Dx_In(Dx_In),
    .n_DMCAB(n_DMCAB), .RUNDMC(RUNDMC), .DMCRDY(DMCRDY), .DMCINT(DMCINT), .DSLOAD(dpcm_ctrl_dsload[0]),
    .DSSTEP(dpcm_ctrl_dsload[1]), .BLOAD(dpcm_ctrl_bload[0]), .BSTEP(dpcm_ctrl_bload[1]),
    .NSTEP(dpcm_ctrl_nstep), .DSTEP(dpcm_ctrl_dstep), .PCM(dpcm_ctrl_pcm), .D4_Out(Dx_Out[4]),
    .D7_Out(Dx_Out[7]));
  DPCM_Output dpcm_out (
    .n_ACLK(n_ACLK), .RES(RES), .W4011(W4011), .CountDown(sbuf_n_bout), .DSTEP(dpcm_ctrl_dstep),
    .Dx_In(Dx_In), .DMC_Out(DMC_Out), .DOUT(dpcm_out_dout));
  DPCM_AddressCounter dpcm_addr_cnt (
    .n_ACLK(n_ACLK), .RES(RES), .DSLOAD(dpcm_ctrl_dsload[0]), .DSSTEP(dpcm_ctrl_dsload[1]),
    .Addr_In(addr_reg_addr_out), .DMC_Addr(DMC_Addr));
  DPCM_ControlReg ctrl_reg (
    .n_ACLK(n_ACLK), .W4010(W4010), .Dx_In(Dx_In), .F_Out(ctrl_reg_f_out), .n_IRQEN(ctrl_reg_n_irqen),
    .LOOPMode(ctrl_reg_loopmode));
  DPCM_Decoder decoder (.Fx(ctrl_reg_f_out), .FR_Out(decoder_fr_out));
  DPCM_SampleCounterReg scnt_in (.n_ACLK(n_ACLK), .W4013(W4013), .Dx_In(Dx_In), .Cnt_Out(scnt_in_cnt_out));
  DPCM_FreqLFSR lfsr (.ACLK(ACLK), .n_ACLK(n_ACLK), .RES(RES), .FR_In(decoder_fr_out), .DFLOAD(sbcnt_n_nout[2]));
  DPCM_SampleCounter scnt (
    .n_ACLK(n_ACLK), .RES(RES), .DSLOAD(dpcm_ctrl_dsload[0]), .DSSTEP(dpcm_ctrl_dsload[1]),
    .Cnt_In(scnt_in_cnt_out), .SOUT(sbcnt_n_nout[1]));
  DPCM_SampleBitCounter sbcnt (.n_ACLK(n_ACLK), .RES(RES), .NSTEP(dpcm_ctrl_nstep), .n_NOUT(sbcnt_n_nout[0]));
  DPCM_SampleBuffer sbuf (
    .n_ACLK(n_ACLK), .RES(RES), .BLOAD(dpcm_ctrl_bload[0]), .BSTEP(dpcm_ctrl_bload[1]), .PCM(dpcm_ctrl_pcm),
    .Dx_In(Dx_In), .n_BOUT(sbuf_n_bout));
endmodule

module DMA (
  input  ACLK,
  input  n_ACLK,
  input  PHI1,
  input  PHI2,
  input  RES,
  input  RnW,
  input  W4014,
  input  [7:0] Dx_In,
  input  RUNDMC,
  input  n_DMC_AB,
  input  DMCRDY,
  input  [15:0] DMC_Addr,
  input  [15:0] CPU_Addr,
  output [15:0] Ax,
  output [7:0] Dx_Out,
  output RW,
  output RDY
);

  wire addr_lo_endcount, dma_ctrl_spr_cpu, dma_ctrl_spr_ppu, dma_ctrl_sprs;
  wire [7:0] addr_hi_spr_addrhi, addr_lo_spr_addrlo;

  SPRDMA_AddrLowCounter addr_lo (
    .n_ACLK(n_ACLK), .Clear(RES), .Step(dma_ctrl_sprs), .Load(W4014), .Value({8{1'b0}}),
    .EndCount(addr_lo_endcount), .SPR_AddrLo(addr_lo_spr_addrlo));
  SPRDMA_AddrHigh addr_hi (.n_ACLK(n_ACLK), .SetAddr(W4014), .Dx_In(Dx_In), .SPR_AddrHi(addr_hi_spr_addrhi));
  SPRDMA_Control dma_ctrl (
    .ACLK(ACLK), .n_ACLK(n_ACLK), .RES(RES), .W4014(W4014), .RUNDMC(RUNDMC), .SPRE(addr_lo_endcount),
    .PHI1(PHI1), .RnW(RnW), .DMCReady(DMCRDY), .SPRS(dma_ctrl_sprs), .RDY(RDY), .SPR_PPU(dma_ctrl_spr_ppu),
    .SPR_CPU(dma_ctrl_spr_cpu));
  Addr_MUX mux (
    .SPR_CPU(dma_ctrl_spr_cpu), .SPR_PPU(dma_ctrl_spr_ppu), .n_DMC_AB(n_DMC_AB), .DMC_Addr(DMC_Addr),
    .SPR_Addr({addr_hi_spr_addrhi, addr_lo_spr_addrlo}), .CPU_Addr(CPU_Addr), .Ax(Ax));
  SPRDMA_Buffer dma_buf (.SPR_PPU(dma_ctrl_spr_ppu), .PHI2(PHI2), .Dx_In(Dx_In), .RnW(RnW), .Dx_Out(Dx_Out), .RW(RW));
endmodule

module CounterBit (
  input  n_ACLK,
  input  Load,
  input  Value,
  input  Clear,
  input  Step,
  input  CarryIn,
  output CarryOut,
  output n_CntOut,
  output CntOut
);

  wire controlled_buffer_1_out, latch1_n_valout, multiplexer_1_out, not_1_out, not_2_out, not_3_out;

  assign controlled_buffer_1_out = Load ? Value : 1'bz;  // Controlled_Buffer controlled_buffer_1
  assign controlled_buffer_1_out = Clear ? 1'b0 : 1'bz;  // Controlled_Buffer controlled_buffer_2
  assign controlled_buffer_1_out = Step ? latch1_n_valout : 1'bz;  // Controlled_Buffer controlled_buffer_3
  assign controlled_buffer_1_out = n_ACLK ? CntOut : 1'bz;  // Controlled_Buffer controlled_buffer_4
  not not_1 (not_1_out, not_2_out);
  not not_2 (not_2_out, not_1_out);
  D_Flip_Flop #(.trigger("high")) d_ff_1 (
    .D(controlled_buffer_1_out), .clk(1'b1), .Q(CntOut), .Qn(n_CntOut));  // open: preset, reset
  Multiplexer multiplexer_1 (.in0(n_CntOut), .in1(CntOut), .out(multiplexer_1_out), .sel(CarryIn));
  DLatch latch1 (.Enable(n_ACLK), .Value(multiplexer_1_out), .n_ValOut(latch1_n_valout));  // open: ValOut
  not not_3 (not_3_out, CarryIn);
  nor nor_1 (CarryOut, not_3_out, n_CntOut);

  // Notes on the sheet:
  //   q
  //   ~q
endmodule

module DownCounterBit (
  input  n_ACLK,
  input  Load,
  input  Value,
  input  Clear,
  input  Step,
  input  CarryIn,
  output CarryOut,
  output n_CntOut,
  output CntOut
);

  wire controlled_buffer_1_out, latch1_n_valout, multiplexer_1_out, not_1_out, not_2_out, not_3_out;

  assign controlled_buffer_1_out = Load ? Value : 1'bz;  // Controlled_Buffer controlled_buffer_1
  assign controlled_buffer_1_out = Clear ? 1'b0 : 1'bz;  // Controlled_Buffer controlled_buffer_2
  assign controlled_buffer_1_out = Step ? latch1_n_valout : 1'bz;  // Controlled_Buffer controlled_buffer_3
  assign controlled_buffer_1_out = n_ACLK ? CntOut : 1'bz;  // Controlled_Buffer controlled_buffer_4
  not not_1 (not_1_out, not_2_out);
  not not_2 (not_2_out, not_1_out);
  D_Flip_Flop #(.trigger("high")) d_ff_1 (
    .D(controlled_buffer_1_out), .clk(1'b1), .Q(CntOut), .Qn(n_CntOut));  // open: preset, reset
  Multiplexer multiplexer_1 (.in0(n_CntOut), .in1(CntOut), .out(multiplexer_1_out), .sel(CarryIn));
  DLatch latch1 (.Enable(n_ACLK), .Value(multiplexer_1_out), .n_ValOut(latch1_n_valout));  // open: ValOut
  not not_3 (not_3_out, CarryIn);
  nor nor_1 (CarryOut, not_3_out, CntOut);

  // Notes on the sheet:
  //   q
  //   ~q
  //   !!!
endmodule

module RevCounterBit (
  input  n_ACLK,
  input  Load,
  input  Value,
  input  Clear,
  input  Step,
  input  CarryIn,
  input  Dec,
  output CarryOut,
  output n_CntOut,
  output CntOut
);

  wire controlled_buffer_1_out, latch1_n_valout, multiplexer_1_out, multiplexer_2_out, not_1_out, not_2_out,
       not_3_out;

  assign controlled_buffer_1_out = Load ? Value : 1'bz;  // Controlled_Buffer controlled_buffer_1
  assign controlled_buffer_1_out = Clear ? 1'b0 : 1'bz;  // Controlled_Buffer controlled_buffer_2
  assign controlled_buffer_1_out = Step ? latch1_n_valout : 1'bz;  // Controlled_Buffer controlled_buffer_3
  assign controlled_buffer_1_out = n_ACLK ? CntOut : 1'bz;  // Controlled_Buffer controlled_buffer_4
  not not_1 (not_1_out, not_2_out);
  not not_2 (not_2_out, not_1_out);
  D_Flip_Flop #(.trigger("high")) d_ff_1 (
    .D(controlled_buffer_1_out), .clk(1'b1), .Q(CntOut), .Qn(n_CntOut));  // open: preset, reset
  Multiplexer multiplexer_1 (.in0(n_CntOut), .in1(CntOut), .out(multiplexer_1_out), .sel(CarryIn));
  DLatch latch1 (.Enable(n_ACLK), .Value(multiplexer_1_out), .n_ValOut(latch1_n_valout));  // open: ValOut
  not not_3 (not_3_out, CarryIn);
  Multiplexer multiplexer_2 (.in0(n_CntOut), .in1(CntOut), .out(multiplexer_2_out), .sel(Dec));
  nor nor_1 (CarryOut, not_3_out, multiplexer_2_out);

  // Notes on the sheet:
  //   q
  //   ~q
endmodule

module SPRDMA_AddrLowCounter (
  input  n_ACLK,
  input  Clear,
  input  Step,
  input  Load,
  input  [7:0] Value,
  output EndCount,
  output [7:0] SPR_AddrLo
);

  Counter8 cnt (
    .n_ACLK(n_ACLK), .Load(Load), .Clear(Clear), .Step(Step), .CarryIn(1'b1), .Value(Value),
    .ValOut(SPR_AddrLo), .CarryOut(EndCount));  // open: n_ValOut
endmodule

module SPRDMA_AddrHigh (
  input  n_ACLK,
  input  SetAddr,
  input  [7:0] Dx_In,
  output [7:0] SPR_AddrHi
);

  wire [7:0] controlled_buffer_1_out, dlatch_x8_1_n_valout, not_1_out;

  assign controlled_buffer_1_out = n_ACLK ? not_1_out : 8'bz;  // Controlled_Buffer controlled_buffer_1
  assign controlled_buffer_1_out = SetAddr ? Dx_In : 8'bz;  // Controlled_Buffer controlled_buffer_2
  assign not_1_out = ~dlatch_x8_1_n_valout;  // NOT_Gate not_1, 8 bits wide
  DLatch_x8 dlatch_x8_1 (
    .Enable(1'b1), .Value(controlled_buffer_1_out), .ValOut(SPR_AddrHi), .n_ValOut(dlatch_x8_1_n_valout));

  // Notes on the sheet:
  //   x8
  //   FFx8
endmodule

module SPRDMA_Control (
  input  ACLK,
  input  n_ACLK,
  input  RES,
  input  W4014,
  input  RUNDMC,
  input  SPRE,
  input  PHI1,
  input  RnW,
  input  DMCReady,
  output SPRS,
  output RDY,
  output SPR_PPU,
  output SPR_CPU
);

  wire and_1_out, dospr_latch_valout, nand_1_out, nand_2_out, nor_1_out, nor_2_out, nor_4_out, nor_5_out,
       nor_6_out, nor_7_out, nor_10_out, nor_11_out, nospr_latch_n_valout, not_1_out, not_2_out, not_3_out,
       not_4_out, not_5_out, spre_latch_valout;

  not not_1 (not_1_out, ACLK);
  DLatch spre_latch (.Enable(n_ACLK), .Value(SPRE), .ValOut(spre_latch_valout));  // open: n_ValOut
  not not_2 (not_2_out, not_1_out);
  not not_3 (not_3_out, nospr_latch_n_valout);
  nor nor_1 (nor_1_out, not_3_out, RES, nor_2_out);
  nor nor_2 (nor_2_out, W4014, nor_1_out);
  nor nor_3 (SPRS, nospr_latch_n_valout, RUNDMC, not_2_out);
  not not_4 (not_4_out, PHI1);
  nor nor_4 (nor_4_out, not_1_out, nor_5_out);
  nor nor_5 (nor_5_out, n_ACLK, nor_4_out);
  and and_1 (and_1_out, SPRS, spre_latch_valout);
  DLatch dospr_latch (.Enable(not_1_out), .Value(nor_2_out), .ValOut(dospr_latch_valout));  // open: n_ValOut
  nand nand_1 (nand_1_out, not_4_out, RnW);
  not not_5 (not_5_out, nor_5_out);
  DLatch nospr_latch (.Enable(n_ACLK), .Value(nor_6_out), .n_ValOut(nospr_latch_n_valout));  // open: ValOut
  nor nor_6 (nor_6_out, and_1_out, RES, nor_7_out);
  nor nor_7 (nor_7_out, nor_11_out, nor_6_out);
  nor nor_8 (SPR_PPU, nospr_latch_n_valout, RUNDMC, not_5_out);
  nor nor_9 (SPR_CPU, nospr_latch_n_valout, RUNDMC, nor_5_out);
  nor nor_10 (nor_10_out, not_3_out, nor_1_out);
  nor nor_11 (nor_11_out, dospr_latch_valout, nand_1_out);
  nand nand_2 (nand_2_out, nor_10_out, DMCReady);
  not not_6 (RDY, nand_2_out);

  // Notes on the sheet:
  //   SPRE
  //   RUNDMC
  //   RES
  //   W4014
  //   Delayed /ACLK
  //   /ACLK
  //   StartDMA
  //   SPRS
  //   RES
  //   PHI1
  //   R/W
  //   RUNDMC
  //   DMADirToggle
  //   StopDMA
  //   DOSPR
  //   Delayed /ACLK
  //   NOSPR
  //   NOSPR
  //   Increment DMA Addr
  //   DOSPR
  //   DMA Buffer -> PPU
  //   RAM -> DMA Buffer
  //   RDY
  //   DMCRDY
endmodule

module SPRDMA_Buffer (
  input  SPR_PPU,
  input  PHI2,
  input  [7:0] Dx_In,
  input  RnW,
  output [7:0] Dx_Out,
  output RW
);

  wire not_1_out, not_2_out, not_3_out;
  wire [7:0] dlatch_x8_1_n_valout, not_4_out;

  not not_1 (not_1_out, RnW);
  nor nor_1 (RW, SPR_PPU, not_1_out);
  not not_2 (not_2_out, SPR_PPU);
  DLatch_x8 dlatch_x8_1 (.Enable(PHI2), .Value(Dx_In), .n_ValOut(dlatch_x8_1_n_valout));  // open: ValOut
  not not_3 (not_3_out, not_2_out);
  assign not_4_out = ~dlatch_x8_1_n_valout;  // NOT_Gate not_4, 8 bits wide
  assign Dx_Out = not_3_out ? not_4_out : 8'bz;  // Controlled_Buffer controlled_buffer_1

  // Notes on the sheet:
  //   PPU/SPR
endmodule

module Addr_MUX (
  input  SPR_CPU,
  input  SPR_PPU,
  input  n_DMC_AB,
  input  [15:0] DMC_Addr,
  input  [15:0] SPR_Addr,
  input  [15:0] CPU_Addr,
  output [15:0] Ax
);

  wire nor_1_out, not_1_out;
  wire [15:0] controlled_buffer_1_out;

  not not_1 (not_1_out, n_DMC_AB);
  nor nor_1 (nor_1_out, SPR_CPU, SPR_PPU, not_1_out);
  assign controlled_buffer_1_out = not_1_out ? DMC_Addr : 16'bz;  // Controlled_Buffer controlled_buffer_1
  assign controlled_buffer_1_out = SPR_CPU ? SPR_Addr : 16'bz;  // Controlled_Buffer controlled_buffer_2
  assign controlled_buffer_1_out = nor_1_out ? CPU_Addr : 16'bz;  // Controlled_Buffer controlled_buffer_3
  assign controlled_buffer_1_out = SPR_PPU ? 16'h2004 : 16'bz;  // Controlled_Buffer controlled_buffer_4
  assign Ax = controlled_buffer_1_out;  // Buffer buffer_1, 16 bits wide

  // Notes on the sheet:
  //   DMC_AB
  //   CPU_AB (default)
endmodule

module DLatch (
  input  Enable,
  input  Value,
  output ValOut,
  output n_ValOut
);

  D_Flip_Flop #(.trigger("high")) d_ff_1 (.D(Value), .clk(Enable), .Q(ValOut), .Qn(n_ValOut));  // open: preset, reset
endmodule

module DLatch_x8 (
  input  Enable,
  input  [7:0] Value,
  output [7:0] ValOut,
  output [7:0] n_ValOut
);

  Register #(.trigger("high")) register_1 (.D(Value), .en(1'b1), .clk(Enable), .Q(ValOut));  // open: clr
  assign n_ValOut = ~ValOut;  // NOT_Gate not_1, 8 bits wide
endmodule

module DPCM_ControlReg (
  input  n_ACLK,
  input  W4010,
  input  [7:0] Dx_In,
  output [3:0] F_Out,
  output n_IRQEN,
  output LOOPMode
);

  RegisterBit registerbit_1 (.n_ACLK(n_ACLK), .Enable(W4010), .Value(Dx_In[0]), .ValOut(F_Out[0]));  // open: n_ValOut
  RegisterBit registerbit_2 (.n_ACLK(n_ACLK), .Enable(W4010), .Value(Dx_In[1]), .ValOut(F_Out[1]));  // open: n_ValOut
  RegisterBit registerbit_3 (.n_ACLK(n_ACLK), .Enable(W4010), .Value(Dx_In[2]), .ValOut(F_Out[2]));  // open: n_ValOut
  RegisterBit registerbit_4 (.n_ACLK(n_ACLK), .Enable(W4010), .Value(Dx_In[3]), .ValOut(F_Out[3]));  // open: n_ValOut
  RegisterBit registerbit_5 (.n_ACLK(n_ACLK), .Enable(W4010), .Value(Dx_In[6]), .ValOut(LOOPMode));  // open: n_ValOut
  RegisterBit registerbit_6 (.n_ACLK(n_ACLK), .Enable(W4010), .Value(Dx_In[7]), .n_ValOut(n_IRQEN));  // open: ValOut
endmodule

module DPCM_IntControl (
  input  RES,
  input  W4015,
  input  n_R4015,
  input  LOOPMod,
  input  AssertInt,
  output D7_Out,
  output DMCINT
);

  wire nor_1_out, nor_2_out, not_1_out;

  nor nor_1 (nor_1_out, AssertInt, nor_2_out);
  nor nor_2 (nor_2_out, nor_1_out, W4015, LOOPMod, RES);
  not not_1 (not_1_out, n_R4015);
  nor nor_3 (DMCINT, nor_1_out, LOOPMod);
  assign D7_Out = not_1_out ? ~nor_1_out : 1'bz;  // Controlled_Inverter controlled_inverter_1
endmodule

module DPCM_EnableControl (
  input  n_ACLK,
  input  RES,
  input  W4015,
  input  n_R4015,
  input  n_IRQEN,
  input  PCMDone,
  input  SOUT,
  input  D4_In,
  output D4_Out,
  output ED1,
  output DMC2,
  output ED2
);

  wire and_1_out, controlled_buffer_1_out, ff_latch_n_valout, not_1_out, not_3_out, or_1_out,
       sout_latch_n_valout;

  assign controlled_buffer_1_out = n_ACLK ? ED2 : 1'bz;  // Controlled_Buffer controlled_buffer_1
  assign controlled_buffer_1_out = W4015 ? D4_In : 1'bz;  // Controlled_Buffer controlled_buffer_2
  or or_1 (or_1_out, ED1, RES);
  DLatch sout_latch (.Enable(n_ACLK), .Value(SOUT), .ValOut(DMC2), .n_ValOut(sout_latch_n_valout));
  not not_1 (not_1_out, PCMDone);
  and and_1 (and_1_out, controlled_buffer_1_out, ~or_1_out);  // AND_Gate
  DLatch ff_latch (.Enable(1'b1), .Value(and_1_out), .n_ValOut(ff_latch_n_valout));  // open: ValOut
  not not_2 (ED2, ff_latch_n_valout);
  nor nor_1 (ED1, n_IRQEN, sout_latch_n_valout, not_1_out);
  not not_3 (not_3_out, n_R4015);
  assign D4_Out = not_3_out ? ~ff_latch_n_valout : 1'bz;  // Controlled_Inverter controlled_inverter_1

  // Notes on the sheet:
  //   DMC1
  //   AssertInt
  //   DMCFinish
  //   DMCEnable
endmodule

module DPCM_DMAControl (
  input  ACLK,
  input  n_ACLK,
  input  PHI1,
  input  RnW,
  input  RES,
  input  nDMAStop,
  input  nDMCEnableDelay,
  output DMCRDY,
  output RUNDMC,
  output n_DMCAB
);

  wire and_1_out, nand_1_out, nor_1_out, nor_2_out, nor_3_out, nor_4_out, nor_5_out, not_1_out, not_2_out,
       not_3_out, run_latch1_n_valout, run_latch1_valout;

  not not_1 (not_1_out, ACLK);
  not not_2 (not_2_out, nDMAStop);
  DLatch run_latch1 (.Enable(not_1_out), .Value(nor_3_out), .ValOut(run_latch1_valout), .n_ValOut(run_latch1_n_valout));
  not not_3 (not_3_out, PHI1);
  DLatch run_latch2 (.Enable(n_ACLK), .Value(run_latch1_n_valout), .n_ValOut(RUNDMC));  // open: ValOut
  nand nand_1 (nand_1_out, not_3_out, RnW);
  nor nor_1 (nor_1_out, nand_1_out, nDMCEnableDelay, not_2_out);
  nor nor_2 (nor_2_out, nor_1_out, nor_3_out);
  nor nor_3 (nor_3_out, nor_2_out, nDMCEnableDelay, RES, not_2_out);
  and and_1 (and_1_out, run_latch1_valout, n_ACLK);
  nor nor_4 (nor_4_out, and_1_out, nor_5_out);
  buf buffer_1 (n_DMCAB, nor_4_out);
  nor nor_5 (nor_5_out, nor_4_out, not_1_out);
  nor nor_6 (DMCRDY, nor_3_out, nor_5_out);

  // Notes on the sheet:
  //   CTRL1
  //   CTRL2
  //   Delayed /ACLK
  //   S
  //   R
  //   DMAStart
endmodule

module DPCM_SampleCounterControl (
  input  ACLK,
  input  n_ACLK,
  input  PCMDone,
  input  DMCFinish,
  input  DMCEnable,
  input  DFLOAD,
  output DSLOAD,
  output DSSTEP,
  output NSTEP,
  output CTRL2
);

  wire and_1_out, en_latch1_n_valout, en_latch2_n_valout, en_latch3_valout, fin_latch_valout, nor_1_out,
       nor_2_out, not_1_out, not_2_out, not_3_out;

  DLatch en_latch1 (.Enable(n_ACLK), .Value(DMCEnable), .n_ValOut(en_latch1_n_valout));  // open: ValOut
  not not_1 (not_1_out, DFLOAD);
  DLatch fin_latch (.Enable(n_ACLK), .Value(DMCFinish), .ValOut(fin_latch_valout));  // open: n_ValOut
  not not_2 (not_2_out, ACLK);
  DLatch en_latch2 (.Enable(not_2_out), .Value(en_latch1_n_valout), .n_ValOut(en_latch2_n_valout));  // open: ValOut
  DLatch en_latch3 (.Enable(n_ACLK), .Value(en_latch2_n_valout), .ValOut(en_latch3_valout), .n_ValOut(CTRL2));
  and and_1 (and_1_out, fin_latch_valout, PCMDone);
  nor nor_1 (nor_1_out, ACLK, en_latch1_n_valout, en_latch3_valout);
  nor nor_2 (nor_2_out, and_1_out, nor_1_out);
  not not_3 (not_3_out, PCMDone);
  not not_4 (DSLOAD, nor_2_out);
  not not_5 (NSTEP, not_1_out);
  nor nor_3 (DSSTEP, not_3_out, nor_1_out, DMCFinish);

  // Notes on the sheet:
  //   DMC1
  //   DMC2
  //   ED2
  //   Edge detector
  //   DMC3
  //   #DMCEnableDelay
endmodule

module DPCM_SampleBufferControl (
  input  ACLK,
  input  n_ACLK,
  input  PHI1,
  input  RES,
  input  LOCK,
  input  DFLOAD,
  input  DOUT,
  input  n_NOUT,
  input  n_DMCAB,
  output BLOAD,
  output BSTEP,
  output PCM,
  output DSTEP,
  output DMC1,
  output CTRL1
);

  wire d_ff_1_q, d_ff_2_qn, dout_latch_valout, nACLK2, nor_2_out, nor_4_out, nor_5_out, nor_6_out, nor_7_out,
       nor_9_out, not_2_out, not_3_out, not_4_out, not_5_out, pcm_latch_valout;

  not not_1 (nACLK2, ACLK);
  not not_2 (not_2_out, DFLOAD);
  nor nor_1 (PCM, PHI1, n_DMCAB);
  not not_3 (not_3_out, d_ff_2_qn);
  DLatch pcm_latch (.Enable(n_ACLK), .Value(nor_6_out), .ValOut(pcm_latch_valout));  // open: n_ValOut
  nor nor_2 (nor_2_out, not_3_out, not_2_out, n_NOUT);
  nor nor_3 (DMC1, pcm_latch_valout, not_4_out);
  not not_4 (not_4_out, nACLK2);
  nor nor_4 (nor_4_out, BLOAD, nor_5_out);
  nor nor_5 (nor_5_out, nor_4_out, nor_2_out, RES);
  DLatch dout_latch (.Enable(n_ACLK), .Value(DOUT), .ValOut(dout_latch_valout));  // open: n_ValOut
  D_Flip_Flop d_ff_1 (.D(nor_4_out), .clk(n_ACLK), .Q(d_ff_1_q));  // open: Qn, preset, reset
  nor nor_6 (nor_6_out, PCM, nor_7_out);
  nor nor_7 (nor_7_out, nor_6_out, DMC1, RES);
  DLatch dstep_latch ();  // open: Enable, Value, ValOut, n_ValOut
  nor nor_8 (CTRL1, PCM, nor_9_out);
  nor nor_9 (nor_9_out, CTRL1, BLOAD, RES);
  nor nor_10 (DSTEP, dout_latch_valout, d_ff_1_q, not_2_out, LOCK);
  not not_5 (not_5_out, n_NOUT);
  D_Flip_Flop d_ff_2 (.D(nor_9_out), .clk(n_ACLK), .Qn(d_ff_2_qn));  // open: Q, preset, reset
  nor nor_11 (BLOAD, d_ff_2_qn, not_2_out, n_NOUT);
  nor nor_12 (BSTEP, not_2_out, not_5_out);
  DLatch stop_latch ();  // open: Enable, Value, ValOut, n_ValOut

  // Notes on the sheet:
  //   Delayed /ACLK
  //   PCM
  //   =
  //   In the schematic, several DLatch are replaced by Posedge DFFs, for simulation purposes.
  //   nDMAStop
  //   =
  //   PCMDone
endmodule

module DPCM_Control (
  input  ACLK,
  input  n_ACLK,
  input  PHI1,
  input  RES,
  input  RnW,
  input  LOCK,
  input  W4015,
  input  n_R4015,
  input  LOOPMod,
  input  n_IRQEN,
  input  DOUT,
  input  n_NOUT,
  input  SOUT,
  input  DFLOAD,
  input  [7:0] Dx_In,
  output n_DMCAB,
  output RUNDMC,
  output DMCRDY,
  output DMCINT,
  output DSLOAD,
  output DSSTEP,
  output BLOAD,
  output BSTEP,
  output NSTEP,
  output DSTEP,
  output PCM,
  output D4_Out,
  output D7_Out
);

  wire enable_ctrl_dmc2, enable_ctrl_ed1, enable_ctrl_ed2, sbuf_ctrl_ctrl1, sbuf_ctrl_dmc1, scnt_ctrl_ctrl2;

  DPCM_IntControl int_ctrl (
    .RES(RES), .W4015(W4015), .n_R4015(n_R4015), .LOOPMod(LOOPMod), .AssertInt(enable_ctrl_ed1),
    .D7_Out(D7_Out), .DMCINT(DMCINT));
  DPCM_EnableControl enable_ctrl (
    .n_ACLK(n_ACLK), .RES(RES), .W4015(W4015), .n_R4015(n_R4015), .n_IRQEN(n_IRQEN),
    .PCMDone(sbuf_ctrl_dmc1), .SOUT(SOUT), .D4_In(Dx_In[4]), .D4_Out(D4_Out), .ED1(enable_ctrl_ed1),
    .DMC2(enable_ctrl_dmc2), .ED2(enable_ctrl_ed2));
  DPCM_DMAControl dma_ctrl (
    .ACLK(ACLK), .n_ACLK(n_ACLK), .PHI1(PHI1), .RnW(RnW), .RES(RES), .nDMAStop(sbuf_ctrl_ctrl1),
    .nDMCEnableDelay(scnt_ctrl_ctrl2), .DMCRDY(DMCRDY), .RUNDMC(RUNDMC), .n_DMCAB(n_DMCAB));
  DPCM_SampleCounterControl scnt_ctrl (
    .ACLK(ACLK), .n_ACLK(n_ACLK), .PCMDone(sbuf_ctrl_dmc1), .DMCFinish(enable_ctrl_dmc2),
    .DMCEnable(enable_ctrl_ed2), .DFLOAD(DFLOAD), .DSLOAD(DSLOAD), .DSSTEP(DSSTEP), .NSTEP(NSTEP),
    .CTRL2(scnt_ctrl_ctrl2));
  DPCM_SampleBufferControl sbuf_ctrl (
    .ACLK(ACLK), .n_ACLK(n_ACLK), .PHI1(PHI1), .RES(RES), .LOCK(LOCK), .DFLOAD(DFLOAD), .DOUT(DOUT),
    .n_NOUT(n_NOUT), .n_DMCAB(n_DMCAB), .BLOAD(BLOAD), .BSTEP(BSTEP), .PCM(PCM), .DSTEP(DSTEP),
    .DMC1(sbuf_ctrl_dmc1), .CTRL1(sbuf_ctrl_ctrl1));
endmodule

module DPCM_SampleCounterReg (
  input  n_ACLK,
  input  W4013,
  input  [7:0] Dx_In,
  output [7:0] Cnt_Out
);

  RegisterBit_x8 cnt_reg (.n_ACLK(n_ACLK), .Enable(W4013), .Value(Dx_In), .ValOut(Cnt_Out));  // open: n_ValOut
endmodule

module DPCM_SampleCounter (
  input  n_ACLK,
  input  RES,
  input  DSLOAD,
  input  DSSTEP,
  input  [7:0] Cnt_In,
  output SOUT
);

  DownCounter12_NoOut scnt (
    .n_ACLK(n_ACLK), .Load(DSLOAD), .Clear(RES), .Step(DSSTEP), .CarryIn(1'b1), .Value({Cnt_In, 4'b0000}),
    .CarryOut(SOUT));
endmodule

module DPCM_SampleBuffer (
  input  n_ACLK,
  input  RES,
  input  BLOAD,
  input  BSTEP,
  input  PCM,
  input  [7:0] Dx_In,
  output n_BOUT
);

  wire shiftreg8_1_shiftout;
  wire [7:0] registerbit_x8_1_n_valout;

  RegisterBit_x8 registerbit_x8_1 (
    .n_ACLK(n_ACLK), .Enable(PCM), .Value(Dx_In), .n_ValOut(registerbit_x8_1_n_valout));  // open: ValOut
  ShiftReg8 shiftreg8_1 (
    .n_ACLK(n_ACLK), .Clear(RES), .Load(BLOAD), .Step(BSTEP), .n_ValueIn(registerbit_x8_1_n_valout),
    .ShiftOut(shiftreg8_1_shiftout));
  not not_1 (n_BOUT, shiftreg8_1_shiftout);

  // Notes on the sheet:
  //   The shift register is loaded with an inverse value, but pushes out the bits in the direct value.
endmodule

module DPCM_SampleBitCounter (
  input  n_ACLK,
  input  RES,
  input  NSTEP,
  output n_NOUT
);

  wire counterbit_1_carryout, counterbit_2_carryout, counterbit_3_carryout;

  CounterBit counterbit_1 (
    .n_ACLK(n_ACLK), .Load(RES), .Value(1'b0), .Clear(RES), .Step(NSTEP), .CarryIn(1'b1),
    .CarryOut(counterbit_1_carryout));  // open: n_CntOut, CntOut
  CounterBit counterbit_2 (
    .n_ACLK(n_ACLK), .Load(RES), .Value(1'b0), .Clear(RES), .Step(NSTEP), .CarryIn(counterbit_1_carryout),
    .CarryOut(counterbit_2_carryout));  // open: n_CntOut, CntOut
  CounterBit counterbit_3 (
    .n_ACLK(n_ACLK), .Load(RES), .Value(1'b0), .Clear(RES), .Step(NSTEP), .CarryIn(counterbit_2_carryout),
    .CarryOut(counterbit_3_carryout));  // open: n_CntOut, CntOut
  DLatch nout_latch (.Enable(n_ACLK), .Value(counterbit_3_carryout), .n_ValOut(n_NOUT));  // open: ValOut
endmodule

module DPCM_Decoder (
  input  [3:0] Fx,
  output [8:0] FR_Out
);

  wire [15:0] pla_4_to_16_pla1_out;

  PLA1 pla_4_to_16 (.Fx(Fx), .PLA1_Out(pla_4_to_16_pla1_out));
  PLA2 pla_16_to_9 (.PLA2_In(pla_4_to_16_pla1_out), .PLA2_Out(FR_Out));
endmodule

module DPCM_FreqLFSR (
  input  ACLK,
  input  n_ACLK,
  input  RES,
  input  [8:0] FR_In,
  output DFLOAD
);

  wire and_1_out, nor_1_out, nor_2_out, nor_3_out, nor_5_out, nor_6_out, nor_7_out, not_1_out, not_2_out,
       not_3_out, not_4_out, not_5_out;
  wire [8:0] lfsr_9_shiftout;

  not not_1 (not_1_out, ACLK);
  not not_2 (not_2_out, nor_7_out);
  and and_1 (and_1_out, lfsr_9_shiftout[0], lfsr_9_shiftout[4]);
  nor nor_1 (nor_1_out, lfsr_9_shiftout[0], lfsr_9_shiftout[4], nor_6_out);
  not not_3 (not_3_out, not_1_out);
  nor nor_2 (nor_2_out, RES, not_2_out);
  nor nor_3 (nor_3_out, and_1_out, RES, nor_1_out);
  nor nor_4 (DFLOAD, not_3_out, not_4_out);
  not not_4 (not_4_out, nor_2_out);
  nor nor_5 (nor_5_out, not_3_out, nor_2_out);
  LFSR9 lfsr_9 (
    .n_ACLK(n_ACLK), .Load(DFLOAD), .Step(nor_5_out), .ShiftIn(nor_3_out), .ValueIn(FR_In),
    .ShiftOut(lfsr_9_shiftout));
  not not_5 (not_5_out, lfsr_9_shiftout[0]);
  nor nor_6 (nor_6_out, lfsr_9_shiftout[0], lfsr_9_shiftout[1], lfsr_9_shiftout[2], lfsr_9_shiftout[3], lfsr_9_shiftout[4], lfsr_9_shiftout[5], lfsr_9_shiftout[6], lfsr_9_shiftout[7], lfsr_9_shiftout[8]);
  nor nor_7 (nor_7_out, not_5_out, lfsr_9_shiftout[1], lfsr_9_shiftout[2], lfsr_9_shiftout[3], lfsr_9_shiftout[4], lfsr_9_shiftout[5], lfsr_9_shiftout[6], lfsr_9_shiftout[7], lfsr_9_shiftout[8]);

  // Notes on the sheet:
  //   Delayed /ACLK
endmodule

module DPCM_AddressReg (
  input  n_ACLK,
  input  W4012,
  input  [7:0] Dx_In,
  output [7:0] Addr_Out
);

  RegisterBit_x8 addr_reg (.n_ACLK(n_ACLK), .Enable(W4012), .Value(Dx_In), .ValOut(Addr_Out));  // open: n_ValOut
endmodule

module DPCM_AddressCounter (
  input  n_ACLK,
  input  RES,
  input  DSLOAD,
  input  DSSTEP,
  input  [7:0] Addr_In,
  output [15:0] DMC_Addr
);

  wire addr_lo_carryout;

  Counter8 addr_lo (
    .n_ACLK(n_ACLK), .Load(DSLOAD), .Clear(RES), .Step(DSSTEP), .CarryIn(1'b1),
    .Value({Addr_In[1:0], {6{1'b0}}}), .ValOut(DMC_Addr[7:0]), .CarryOut(addr_lo_carryout));  // open: n_ValOut
  Counter7 addr_hi (
    .n_ACLK(n_ACLK), .Load(DSLOAD), .Clear(RES), .Step(DSSTEP), .CarryIn(addr_lo_carryout),
    .Value({1'b1, Addr_In[7:2]}), .ValOut(DMC_Addr[14:8]));  // open: n_ValOut, CarryOut

  assign DMC_Addr[15] = 1'b1;
endmodule

module DPCM_Output (
  input  n_ACLK,
  input  RES,
  input  W4011,
  input  CountDown,
  input  DSTEP,
  input  [7:0] Dx_In,
  output [6:0] DMC_Out,
  output DOUT
);

  RevCounter6 revcounter6_1 (
    .n_ACLK(n_ACLK), .Load(W4011), .Clear(RES), .Step(DSTEP), .CarryIn(1'b1), .Dec(CountDown),
    .Value(Dx_In[6:1]), .ValOut(DMC_Out[6:1]), .CarryOut(DOUT));  // open: n_ValOut
  RegisterBit registerbit_1 (.n_ACLK(n_ACLK), .Enable(W4011), .Value(Dx_In[0]), .ValOut(DMC_Out[0]));  // open: n_ValOut

  // Notes on the sheet:
  //   n_BOUT
endmodule

module Counter8 (
  input  n_ACLK,
  input  Load,
  input  Clear,
  input  Step,
  input  CarryIn,
  input  [7:0] Value,
  output [7:0] ValOut,
  output [7:0] n_ValOut,
  output CarryOut
);

  wire counterbit_1_carryout, counterbit_2_carryout, counterbit_3_carryout, counterbit_4_carryout,
       counterbit_5_carryout, counterbit_6_carryout, counterbit_7_carryout;

  CounterBit counterbit_1 (
    .n_ACLK(n_ACLK), .Load(Load), .Value(Value[0]), .Clear(Clear), .Step(Step), .CarryIn(CarryIn),
    .CarryOut(counterbit_1_carryout), .n_CntOut(n_ValOut[0]), .CntOut(ValOut[0]));
  CounterBit counterbit_2 (
    .n_ACLK(n_ACLK), .Load(Load), .Value(Value[1]), .Clear(Clear), .Step(Step),
    .CarryIn(counterbit_1_carryout), .CarryOut(counterbit_2_carryout), .n_CntOut(n_ValOut[1]),
    .CntOut(ValOut[1]));
  CounterBit counterbit_3 (
    .n_ACLK(n_ACLK), .Load(Load), .Value(Value[2]), .Clear(Clear), .Step(Step),
    .CarryIn(counterbit_2_carryout), .CarryOut(counterbit_3_carryout), .n_CntOut(n_ValOut[2]),
    .CntOut(ValOut[2]));
  CounterBit counterbit_4 (
    .n_ACLK(n_ACLK), .Load(Load), .Value(Value[3]), .Clear(Clear), .Step(Step),
    .CarryIn(counterbit_3_carryout), .CarryOut(counterbit_4_carryout), .n_CntOut(n_ValOut[3]),
    .CntOut(ValOut[3]));
  CounterBit counterbit_5 (
    .n_ACLK(n_ACLK), .Load(Load), .Value(Value[4]), .Clear(Clear), .Step(Step),
    .CarryIn(counterbit_4_carryout), .CarryOut(counterbit_5_carryout), .n_CntOut(n_ValOut[4]),
    .CntOut(ValOut[4]));
  CounterBit counterbit_6 (
    .n_ACLK(n_ACLK), .Load(Load), .Value(Value[5]), .Clear(Clear), .Step(Step),
    .CarryIn(counterbit_5_carryout), .CarryOut(counterbit_6_carryout), .n_CntOut(n_ValOut[5]),
    .CntOut(ValOut[5]));
  CounterBit counterbit_7 (
    .n_ACLK(n_ACLK), .Load(Load), .Value(Value[6]), .Clear(Clear), .Step(Step),
    .CarryIn(counterbit_6_carryout), .CarryOut(counterbit_7_carryout), .n_CntOut(n_ValOut[6]),
    .CntOut(ValOut[6]));
  CounterBit counterbit_8 (
    .n_ACLK(n_ACLK), .Load(Load), .Value(Value[7]), .Clear(Clear), .Step(Step),
    .CarryIn(counterbit_7_carryout), .CarryOut(CarryOut), .n_CntOut(n_ValOut[7]), .CntOut(ValOut[7]));
endmodule

module Counter7 (
  input  n_ACLK,
  input  Load,
  input  Clear,
  input  Step,
  input  CarryIn,
  input  [6:0] Value,
  output [6:0] ValOut,
  output [6:0] n_ValOut,
  output CarryOut
);

  wire counterbit_1_carryout, counterbit_2_carryout, counterbit_3_carryout, counterbit_4_carryout,
       counterbit_5_carryout, counterbit_6_carryout;

  CounterBit counterbit_1 (
    .n_ACLK(n_ACLK), .Load(Load), .Value(Value[0]), .Clear(Clear), .Step(Step), .CarryIn(CarryIn),
    .CarryOut(counterbit_1_carryout), .n_CntOut(n_ValOut[0]), .CntOut(ValOut[0]));
  CounterBit counterbit_2 (
    .n_ACLK(n_ACLK), .Load(Load), .Value(Value[1]), .Clear(Clear), .Step(Step),
    .CarryIn(counterbit_1_carryout), .CarryOut(counterbit_2_carryout), .n_CntOut(n_ValOut[1]),
    .CntOut(ValOut[1]));
  CounterBit counterbit_3 (
    .n_ACLK(n_ACLK), .Load(Load), .Value(Value[2]), .Clear(Clear), .Step(Step),
    .CarryIn(counterbit_2_carryout), .CarryOut(counterbit_3_carryout), .n_CntOut(n_ValOut[2]),
    .CntOut(ValOut[2]));
  CounterBit counterbit_4 (
    .n_ACLK(n_ACLK), .Load(Load), .Value(Value[3]), .Clear(Clear), .Step(Step),
    .CarryIn(counterbit_3_carryout), .CarryOut(counterbit_4_carryout), .n_CntOut(n_ValOut[3]),
    .CntOut(ValOut[3]));
  CounterBit counterbit_5 (
    .n_ACLK(n_ACLK), .Load(Load), .Value(Value[4]), .Clear(Clear), .Step(Step),
    .CarryIn(counterbit_4_carryout), .CarryOut(counterbit_5_carryout), .n_CntOut(n_ValOut[4]),
    .CntOut(ValOut[4]));
  CounterBit counterbit_6 (
    .n_ACLK(n_ACLK), .Load(Load), .Value(Value[5]), .Clear(Clear), .Step(Step),
    .CarryIn(counterbit_5_carryout), .CarryOut(counterbit_6_carryout), .n_CntOut(n_ValOut[5]),
    .CntOut(ValOut[5]));
  CounterBit counterbit_7 (
    .n_ACLK(n_ACLK), .Load(Load), .Value(Value[6]), .Clear(Clear), .Step(Step),
    .CarryIn(counterbit_6_carryout), .CarryOut(CarryOut), .n_CntOut(n_ValOut[6]), .CntOut(ValOut[6]));
endmodule

module DownCounter12_NoOut (
  input  n_ACLK,
  input  Load,
  input  Clear,
  input  Step,
  input  CarryIn,
  input  [11:0] Value,
  output CarryOut
);

  wire downcounterbit_1_carryout, downcounterbit_2_carryout, downcounterbit_3_carryout,
       downcounterbit_4_carryout, downcounterbit_5_carryout, downcounterbit_6_carryout,
       downcounterbit_7_carryout, downcounterbit_8_carryout, downcounterbit_9_carryout,
       downcounterbit_10_carryout, downcounterbit_11_carryout;

  DownCounterBit downcounterbit_1 (
    .n_ACLK(n_ACLK), .Load(Load), .Value(Value[0]), .Clear(Clear), .Step(Step), .CarryIn(CarryIn),
    .CarryOut(downcounterbit_1_carryout));  // open: n_CntOut, CntOut
  DownCounterBit downcounterbit_2 (
    .n_ACLK(n_ACLK), .Load(Load), .Value(Value[1]), .Clear(Clear), .Step(Step),
    .CarryIn(downcounterbit_1_carryout), .CarryOut(downcounterbit_2_carryout));  // open: n_CntOut, CntOut
  DownCounterBit downcounterbit_3 (
    .n_ACLK(n_ACLK), .Load(Load), .Value(Value[2]), .Clear(Clear), .Step(Step),
    .CarryIn(downcounterbit_2_carryout), .CarryOut(downcounterbit_3_carryout));  // open: n_CntOut, CntOut
  DownCounterBit downcounterbit_4 (
    .n_ACLK(n_ACLK), .Load(Load), .Value(Value[3]), .Clear(Clear), .Step(Step),
    .CarryIn(downcounterbit_3_carryout), .CarryOut(downcounterbit_4_carryout));  // open: n_CntOut, CntOut
  DownCounterBit downcounterbit_5 (
    .n_ACLK(n_ACLK), .Load(Load), .Value(Value[4]), .Clear(Clear), .Step(Step),
    .CarryIn(downcounterbit_4_carryout), .CarryOut(downcounterbit_5_carryout));  // open: n_CntOut, CntOut
  DownCounterBit downcounterbit_6 (
    .n_ACLK(n_ACLK), .Load(Load), .Value(Value[5]), .Clear(Clear), .Step(Step),
    .CarryIn(downcounterbit_5_carryout), .CarryOut(downcounterbit_6_carryout));  // open: n_CntOut, CntOut
  DownCounterBit downcounterbit_7 (
    .n_ACLK(n_ACLK), .Load(Load), .Value(Value[6]), .Clear(Clear), .Step(Step),
    .CarryIn(downcounterbit_6_carryout), .CarryOut(downcounterbit_7_carryout));  // open: n_CntOut, CntOut
  DownCounterBit downcounterbit_8 (
    .n_ACLK(n_ACLK), .Load(Load), .Value(Value[7]), .Clear(Clear), .Step(Step),
    .CarryIn(downcounterbit_7_carryout), .CarryOut(downcounterbit_8_carryout));  // open: n_CntOut, CntOut
  DownCounterBit downcounterbit_9 (
    .n_ACLK(n_ACLK), .Load(Load), .Value(Value[8]), .Clear(Clear), .Step(Step),
    .CarryIn(downcounterbit_8_carryout), .CarryOut(downcounterbit_9_carryout));  // open: n_CntOut, CntOut
  DownCounterBit downcounterbit_10 (
    .n_ACLK(n_ACLK), .Load(Load), .Value(Value[9]), .Clear(Clear), .Step(Step),
    .CarryIn(downcounterbit_9_carryout), .CarryOut(downcounterbit_10_carryout));  // open: n_CntOut, CntOut
  DownCounterBit downcounterbit_11 (
    .n_ACLK(n_ACLK), .Load(Load), .Value(Value[10]), .Clear(Clear), .Step(Step),
    .CarryIn(downcounterbit_10_carryout), .CarryOut(downcounterbit_11_carryout));  // open: n_CntOut, CntOut
  DownCounterBit downcounterbit_12 (
    .n_ACLK(n_ACLK), .Load(Load), .Value(Value[11]), .Clear(Clear), .Step(Step),
    .CarryIn(downcounterbit_11_carryout), .CarryOut(CarryOut));  // open: n_CntOut, CntOut
endmodule

module RegisterBit (
  input  n_ACLK,
  input  Enable,
  input  Value,
  output ValOut,
  output n_ValOut
);

  wire controlled_buffer_1_out;

  assign controlled_buffer_1_out = n_ACLK ? ValOut : 1'bz;  // Controlled_Buffer controlled_buffer_1
  assign controlled_buffer_1_out = Enable ? Value : 1'bz;  // Controlled_Buffer controlled_buffer_2
  DLatch ff_latch (.Enable(1'b1), .Value(controlled_buffer_1_out), .n_ValOut(n_ValOut));  // open: ValOut
  not not_1 (ValOut, n_ValOut);
endmodule

module RegisterBit_x8 (
  input  n_ACLK,
  input  Enable,
  input  [7:0] Value,
  output [7:0] ValOut,
  output [7:0] n_ValOut
);

  RegisterBit registerbit_1 (
    .n_ACLK(n_ACLK), .Enable(Enable), .Value(Value[0]), .ValOut(ValOut[0]), .n_ValOut(n_ValOut[0]));
  RegisterBit registerbit_2 (
    .n_ACLK(n_ACLK), .Enable(Enable), .Value(Value[1]), .ValOut(ValOut[1]), .n_ValOut(n_ValOut[1]));
  RegisterBit registerbit_3 (
    .n_ACLK(n_ACLK), .Enable(Enable), .Value(Value[2]), .ValOut(ValOut[2]), .n_ValOut(n_ValOut[2]));
  RegisterBit registerbit_4 (
    .n_ACLK(n_ACLK), .Enable(Enable), .Value(Value[3]), .ValOut(ValOut[3]), .n_ValOut(n_ValOut[3]));
  RegisterBit registerbit_5 (
    .n_ACLK(n_ACLK), .Enable(Enable), .Value(Value[4]), .ValOut(ValOut[4]), .n_ValOut(n_ValOut[4]));
  RegisterBit registerbit_6 (
    .n_ACLK(n_ACLK), .Enable(Enable), .Value(Value[5]), .ValOut(ValOut[5]), .n_ValOut(n_ValOut[5]));
  RegisterBit registerbit_7 (
    .n_ACLK(n_ACLK), .Enable(Enable), .Value(Value[6]), .ValOut(ValOut[6]), .n_ValOut(n_ValOut[6]));
  RegisterBit registerbit_8 (
    .n_ACLK(n_ACLK), .Enable(Enable), .Value(Value[7]), .ValOut(ValOut[7]), .n_ValOut(n_ValOut[7]));
endmodule

module RegisterBitRes (
  input  Res,
  input  n_ACLK,
  input  Enable,
  input  Value,
  output ValOut,
  output n_ValOut
);

  wire controlled_buffer_1_out;

  assign controlled_buffer_1_out = Res ? 1'b0 : 1'bz;  // Controlled_Buffer controlled_buffer_1
  assign controlled_buffer_1_out = n_ACLK ? ValOut : 1'bz;  // Controlled_Buffer controlled_buffer_2
  assign controlled_buffer_1_out = Enable ? Value : 1'bz;  // Controlled_Buffer controlled_buffer_3
  DLatch ff_latch (.Enable(1'b1), .Value(controlled_buffer_1_out), .n_ValOut(n_ValOut));  // open: ValOut
  not not_1 (ValOut, n_ValOut);
endmodule

module SRBit (
  input  n_ACLK,
  input  Clear,
  input  Load,
  input  Step,
  input  n_ValueIn,
  input  ShiftIn,
  output ShiftOut
);

  wire controlled_buffer_1_out, dlatch_1_n_valout, not_1_out;

  DLatch dlatch_1 (.Enable(n_ACLK), .Value(ShiftIn), .n_ValOut(dlatch_1_n_valout));  // open: ValOut
  assign controlled_buffer_1_out = Clear ? 1'b0 : 1'bz;  // Controlled_Buffer controlled_buffer_1
  assign controlled_buffer_1_out = Load ? n_ValueIn : 1'bz;  // Controlled_Buffer controlled_buffer_2
  assign controlled_buffer_1_out = Step ? dlatch_1_n_valout : 1'bz;  // Controlled_Buffer controlled_buffer_3
  assign controlled_buffer_1_out = n_ACLK ? not_1_out : 1'bz;  // Controlled_Buffer controlled_buffer_4
  DLatch dlatch_2 (.Enable(1'b1), .Value(controlled_buffer_1_out), .n_ValOut(ShiftOut));  // open: ValOut
  not not_1 (not_1_out, ShiftOut);
endmodule

module ShiftReg8 (
  input  n_ACLK,
  input  Clear,
  input  Load,
  input  Step,
  input  [7:0] n_ValueIn,
  output ShiftOut
);

  wire srbit_1_shiftout, srbit_2_shiftout, srbit_3_shiftout, srbit_4_shiftout, srbit_5_shiftout,
       srbit_6_shiftout, srbit_7_shiftout;

  SRBit srbit_1 (
    .n_ACLK(n_ACLK), .Clear(Clear), .Load(Load), .Step(Step), .n_ValueIn(n_ValueIn[7]), .ShiftIn(1'b0),
    .ShiftOut(srbit_1_shiftout));
  SRBit srbit_2 (
    .n_ACLK(n_ACLK), .Clear(Clear), .Load(Load), .Step(Step), .n_ValueIn(n_ValueIn[6]),
    .ShiftIn(srbit_1_shiftout), .ShiftOut(srbit_2_shiftout));
  SRBit srbit_3 (
    .n_ACLK(n_ACLK), .Clear(Clear), .Load(Load), .Step(Step), .n_ValueIn(n_ValueIn[5]),
    .ShiftIn(srbit_2_shiftout), .ShiftOut(srbit_3_shiftout));
  SRBit srbit_4 (
    .n_ACLK(n_ACLK), .Clear(Clear), .Load(Load), .Step(Step), .n_ValueIn(n_ValueIn[4]),
    .ShiftIn(srbit_3_shiftout), .ShiftOut(srbit_4_shiftout));
  SRBit srbit_5 (
    .n_ACLK(n_ACLK), .Clear(Clear), .Load(Load), .Step(Step), .n_ValueIn(n_ValueIn[3]),
    .ShiftIn(srbit_4_shiftout), .ShiftOut(srbit_5_shiftout));
  SRBit srbit_6 (
    .n_ACLK(n_ACLK), .Clear(Clear), .Load(Load), .Step(Step), .n_ValueIn(n_ValueIn[2]),
    .ShiftIn(srbit_5_shiftout), .ShiftOut(srbit_6_shiftout));
  SRBit srbit_7 (
    .n_ACLK(n_ACLK), .Clear(Clear), .Load(Load), .Step(Step), .n_ValueIn(n_ValueIn[1]),
    .ShiftIn(srbit_6_shiftout), .ShiftOut(srbit_7_shiftout));
  SRBit srbit_8 (
    .n_ACLK(n_ACLK), .Clear(Clear), .Load(Load), .Step(Step), .n_ValueIn(n_ValueIn[0]),
    .ShiftIn(srbit_7_shiftout), .ShiftOut(ShiftOut));
endmodule

module PLA1 (
  input  [3:0] Fx,
  output [15:0] PLA1_Out
);

  wire not_1_out, not_2_out, not_3_out, not_4_out;

  Demultiplexer #(.select(4)) demultiplexer_1 (
    .in(1'b1), .sel(Fx));  // open: out0, out1, out2, out3, out4, out5, out6, out7, out8, out9, out10, out11, out12, out13, out14, out15
  not not_1 (not_1_out, Fx[3]);
  not not_2 (not_2_out, Fx[2]);
  not not_3 (not_3_out, Fx[1]);
  not not_4 (not_4_out, Fx[0]);
  nor nor_1 (PLA1_Out[15], not_1_out, not_2_out, not_3_out, not_4_out);
  nor nor_2 (PLA1_Out[14], not_1_out, not_2_out, not_3_out, Fx[0]);
  nor nor_3 (PLA1_Out[13], not_1_out, not_2_out, Fx[1], not_4_out);
  nor nor_4 (PLA1_Out[12], not_1_out, not_2_out, Fx[1], Fx[0]);
  nor nor_5 (PLA1_Out[11], not_1_out, Fx[2], not_3_out, not_4_out);
  nor nor_6 (PLA1_Out[10], not_1_out, Fx[2], not_3_out, Fx[0]);
  nor nor_7 (PLA1_Out[9], not_1_out, Fx[2], Fx[1], not_4_out);
  nor nor_8 (PLA1_Out[8], not_1_out, Fx[2], Fx[1], Fx[0]);
  nor nor_9 (PLA1_Out[7], Fx[3], not_2_out, not_3_out, not_4_out);
  nor nor_10 (PLA1_Out[6], Fx[3], not_2_out, not_3_out, Fx[0]);
  nor nor_11 (PLA1_Out[5], Fx[3], not_2_out, Fx[1], not_4_out);
  nor nor_12 (PLA1_Out[4], Fx[3], not_2_out, Fx[1], Fx[0]);
  nor nor_13 (PLA1_Out[3], Fx[3], Fx[2], not_3_out, not_4_out);
  nor nor_14 (PLA1_Out[2], Fx[3], Fx[2], not_3_out, Fx[0]);
  nor nor_15 (PLA1_Out[1], Fx[3], Fx[2], Fx[1], not_4_out);
  nor nor_16 (PLA1_Out[0], Fx[3], Fx[2], Fx[1], Fx[0]);

  // Notes on the sheet:
  //   DMX 4-to-16
endmodule

module PLA2 (
  input  [15:0] PLA2_In,
  output [8:0] PLA2_Out
);

  nor nor_1 (PLA2_Out[0], PLA2_In[15], PLA2_In[14], PLA2_In[9], PLA2_In[4], PLA2_In[1]);
  nor nor_2 (PLA2_Out[1], PLA2_In[13], PLA2_In[12], PLA2_In[11], PLA2_In[10], PLA2_In[9], PLA2_In[8], PLA2_In[7], PLA2_In[6]);
  nor nor_3 (PLA2_Out[2], PLA2_In[13], PLA2_In[11], PLA2_In[10], PLA2_In[8], PLA2_In[7], PLA2_In[3], PLA2_In[2], PLA2_In[1], PLA2_In[0]);
  nor nor_4 (PLA2_Out[3], PLA2_In[15], PLA2_In[10], PLA2_In[7], PLA2_In[2], PLA2_In[0]);
  nor nor_5 (PLA2_Out[4], PLA2_In[14], PLA2_In[13], PLA2_In[12], PLA2_In[8], PLA2_In[4], PLA2_In[2], PLA2_In[1]);
  nor nor_6 (PLA2_Out[5], PLA2_In[15], PLA2_In[14], PLA2_In[13], PLA2_In[12], PLA2_In[9], PLA2_In[8], PLA2_In[7], PLA2_In[3], PLA2_In[2], PLA2_In[1]);
  nor nor_7 (PLA2_Out[6], PLA2_In[14], PLA2_In[13], PLA2_In[12], PLA2_In[8], PLA2_In[5], PLA2_In[1]);
  nor nor_8 (PLA2_Out[7], PLA2_In[15], PLA2_In[8], PLA2_In[6], PLA2_In[5], PLA2_In[2], PLA2_In[0]);
  nor nor_9 (PLA2_Out[8], PLA2_In[12], PLA2_In[11], PLA2_In[10], PLA2_In[9], PLA2_In[8], PLA2_In[6], PLA2_In[5], PLA2_In[3], PLA2_In[1]);
endmodule

module LFSRBit (
  input  n_ACLK,
  input  Load,
  input  Step,
  input  ValueIn,
  input  ShiftIn,
  output ShiftOut
);

  wire controlled_buffer_1_out, d_ff_1_qn, or_1_out;

  or or_1 (or_1_out, Load, Step);
  assign controlled_buffer_1_out = Load ? ValueIn : 1'bz;  // Controlled_Buffer controlled_buffer_1
  assign controlled_buffer_1_out = Step ? ShiftIn : 1'bz;  // Controlled_Buffer controlled_buffer_2
  D_Flip_Flop d_ff_1 (.D(controlled_buffer_1_out), .clk(or_1_out), .Qn(d_ff_1_qn));  // open: Q, preset, reset
  D_Flip_Flop d_ff_2 (.D(d_ff_1_qn), .clk(n_ACLK), .Qn(ShiftOut));  // open: Q, preset, reset
endmodule

module LFSR9 (
  input  n_ACLK,
  input  Load,
  input  Step,
  input  ShiftIn,
  input  [8:0] ValueIn,
  output [8:0] ShiftOut
);

  LFSRBit msb (
    .n_ACLK(n_ACLK), .Load(Load), .Step(Step), .ValueIn(ValueIn[8]), .ShiftIn(ShiftIn), .ShiftOut(ShiftOut[8]));
  LFSRBit lfsrbit_1 (
    .n_ACLK(n_ACLK), .Load(Load), .Step(Step), .ValueIn(ValueIn[7]), .ShiftIn(ShiftOut[8]),
    .ShiftOut(ShiftOut[7]));
  LFSRBit lfsrbit_2 (
    .n_ACLK(n_ACLK), .Load(Load), .Step(Step), .ValueIn(ValueIn[6]), .ShiftIn(ShiftOut[7]),
    .ShiftOut(ShiftOut[6]));
  LFSRBit lfsrbit_3 (
    .n_ACLK(n_ACLK), .Load(Load), .Step(Step), .ValueIn(ValueIn[5]), .ShiftIn(ShiftOut[6]),
    .ShiftOut(ShiftOut[5]));
  LFSRBit lfsrbit_4 (
    .n_ACLK(n_ACLK), .Load(Load), .Step(Step), .ValueIn(ValueIn[4]), .ShiftIn(ShiftOut[5]),
    .ShiftOut(ShiftOut[4]));
  LFSRBit lfsrbit_5 (
    .n_ACLK(n_ACLK), .Load(Load), .Step(Step), .ValueIn(ValueIn[3]), .ShiftIn(ShiftOut[4]),
    .ShiftOut(ShiftOut[3]));
  LFSRBit lfsrbit_6 (
    .n_ACLK(n_ACLK), .Load(Load), .Step(Step), .ValueIn(ValueIn[2]), .ShiftIn(ShiftOut[3]),
    .ShiftOut(ShiftOut[2]));
  LFSRBit lfsrbit_7 (
    .n_ACLK(n_ACLK), .Load(Load), .Step(Step), .ValueIn(ValueIn[1]), .ShiftIn(ShiftOut[2]),
    .ShiftOut(ShiftOut[1]));
  LFSRBit lsb (
    .n_ACLK(n_ACLK), .Load(Load), .Step(Step), .ValueIn(ValueIn[0]), .ShiftIn(ShiftOut[1]),
    .ShiftOut(ShiftOut[0]));
endmodule

module RevCounter6 (
  input  n_ACLK,
  input  Load,
  input  Clear,
  input  Step,
  input  CarryIn,
  input  Dec,
  input  [5:0] Value,
  output [5:0] ValOut,
  output [5:0] n_ValOut,
  output CarryOut
);

  wire revcounterbit_1_carryout, revcounterbit_2_carryout, revcounterbit_3_carryout,
       revcounterbit_4_carryout, revcounterbit_5_carryout;

  RevCounterBit revcounterbit_1 (
    .n_ACLK(n_ACLK), .Load(Load), .Value(Value[0]), .Clear(Clear), .Step(Step), .CarryIn(CarryIn), .Dec(Dec),
    .CarryOut(revcounterbit_1_carryout), .n_CntOut(n_ValOut[0]), .CntOut(ValOut[0]));
  RevCounterBit revcounterbit_2 (
    .n_ACLK(n_ACLK), .Load(Load), .Value(Value[1]), .Clear(Clear), .Step(Step),
    .CarryIn(revcounterbit_1_carryout), .Dec(Dec), .CarryOut(revcounterbit_2_carryout),
    .n_CntOut(n_ValOut[1]), .CntOut(ValOut[1]));
  RevCounterBit revcounterbit_3 (
    .n_ACLK(n_ACLK), .Load(Load), .Value(Value[2]), .Clear(Clear), .Step(Step),
    .CarryIn(revcounterbit_2_carryout), .Dec(Dec), .CarryOut(revcounterbit_3_carryout),
    .n_CntOut(n_ValOut[2]), .CntOut(ValOut[2]));
  RevCounterBit revcounterbit_4 (
    .n_ACLK(n_ACLK), .Load(Load), .Value(Value[3]), .Clear(Clear), .Step(Step),
    .CarryIn(revcounterbit_3_carryout), .Dec(Dec), .CarryOut(revcounterbit_4_carryout),
    .n_CntOut(n_ValOut[3]), .CntOut(ValOut[3]));
  RevCounterBit revcounterbit_5 (
    .n_ACLK(n_ACLK), .Load(Load), .Value(Value[4]), .Clear(Clear), .Step(Step),
    .CarryIn(revcounterbit_4_carryout), .Dec(Dec), .CarryOut(revcounterbit_5_carryout),
    .n_CntOut(n_ValOut[4]), .CntOut(ValOut[4]));
  RevCounterBit revcounterbit_6 (
    .n_ACLK(n_ACLK), .Load(Load), .Value(Value[5]), .Clear(Clear), .Step(Step),
    .CarryIn(revcounterbit_5_carryout), .Dec(Dec), .CarryOut(CarryOut), .n_CntOut(n_ValOut[5]),
    .CntOut(ValOut[5]));
endmodule

module Core (
  input  PHI0,
  input  n_NMI,
  input  n_IRQ,
  input  n_RES,
  input  RDY,
  input  [7:0] D_in,
  output PHI1,
  output PHI2,
  output RnW,
  output SYNC,
  output [15:0] Ax,
  output [7:0] D_Out
);

  MOS_6502 core (
    .n_RES(n_RES), .SO(1'b1), .PHI0(PHI0), .D0(D_in[0]), .D1(D_in[1]), .D2(D_in[2]), .D3(D_in[3]),
    .D4(D_in[4]), .D5(D_in[5]), .D6(D_in[6]), .D7(D_in[7]), .n_NMI(n_NMI), .n_IRQ(n_IRQ), .RDY(RDY),
    .PHI2(PHI2), .RnW(RnW), .D_out0(D_Out[0]), .D_out1(D_Out[1]), .D_out2(D_Out[2]), .D_out3(D_Out[3]),
    .D_out4(D_Out[4]), .D_out5(D_Out[5]), .D_out6(D_Out[6]), .D_out7(D_Out[7]), .A8(Ax[8]), .A9(Ax[9]),
    .A10(Ax[10]), .A11(Ax[11]), .A12(Ax[12]), .A13(Ax[13]), .A14(Ax[14]), .A0(Ax[0]), .A1(Ax[1]), .A2(Ax[2]),
    .A3(Ax[3]), .A4(Ax[4]), .A5(Ax[5]), .A6(Ax[6]), .A7(Ax[7]), .SYNC(SYNC), .A15(Ax[15]), .PHI1(PHI1));
endmodule

module SoundGenerators (
  input  PHI1,
  input  PHI2,
  input  ACLK,
  input  n_ACLK,
  input  n_LFO1,
  input  n_LFO2,
  input  RES,
  input  [28:0] RegOps,
  input  [7:0] D_In,
  input  [15:0] CPU_Ax,
  input  CPU_RnW,
  input  LOCK,
  output DMCINT,
  output RDY,
  output APU_RW,
  output [15:0] APU_Ax,
  output [7:0] D_Out,
  output [7:0] AUX_A,
  output [14:0] AUX_B
);

  wire dpcm_dmcrdy, dpcm_n_dmcab, dpcm_rundmc, lc_nornd, lc_nosqa, lc_nosqb, lc_notri, rnd_rnd_lc, sqa_sq_lc,
       sqb_sq_lc, tria_tri_lc;
  wire [15:0] dpcm_dmc_addr;

  LengthCounters lc (
    .ACLK(ACLK), .n_ACLK(n_ACLK), .RES(RES), .W4015(RegOps[22]), .n_R4015(RegOps[2]), .W4003(RegOps[17]),
    .W4007(RegOps[18]), .W400B(RegOps[9]), .W400F(RegOps[24]), .DB_In(D_In), .n_LFO2(n_LFO2),
    .SQA_LC(sqa_sq_lc), .SQB_LC(sqb_sq_lc), .TRI_LC(tria_tri_lc), .RND_LC(rnd_rnd_lc), .DB_Out(D_Out),
    .NOSQA(lc_nosqa), .NOSQB(lc_nosqb), .NOTRI(lc_notri), .NORND(lc_nornd));
  SQUARE sqa (
    .ACLK(ACLK), .n_ACLK(n_ACLK), .RES(RES), .WR0(RegOps[21]), .WR1(RegOps[4]), .WR2(RegOps[3]),
    .WR3(RegOps[17]), .n_LFO1(n_LFO1), .n_LFO2(n_LFO2), .NOSQ(lc_nosqa), .LOCK(LOCK), .CarryMode(1'b1),
    .DB_in(D_In), .SQ_LC(sqa_sq_lc), .SQ_Out(AUX_A[3:0]));
  SQUARE sqb (
    .ACLK(ACLK), .n_ACLK(n_ACLK), .RES(RES), .WR0(RegOps[19]), .WR1(RegOps[5]), .WR2(RegOps[6]),
    .WR3(RegOps[18]), .n_LFO1(n_LFO1), .n_LFO2(n_LFO2), .NOSQ(lc_nosqb), .LOCK(LOCK), .CarryMode(1'b0),
    .DB_in(D_In), .SQ_LC(sqb_sq_lc), .SQ_Out(AUX_A[7:4]));
  DMC dpcm (
    .ACLK(ACLK), .n_ACLK(n_ACLK), .PHI1(PHI1), .RES(RES), .RnW(CPU_RnW), .LOCK(LOCK), .W4010(RegOps[13]),
    .W4011(RegOps[23]), .W4012(RegOps[12]), .W4013(RegOps[11]), .W4015(RegOps[22]), .n_R4015(RegOps[2]),
    .Dx_In(D_In), .n_DMCAB(dpcm_n_dmcab), .RUNDMC(dpcm_rundmc), .DMCRDY(dpcm_dmcrdy), .DMCINT(DMCINT),
    .Dx_Out(D_Out), .DMC_Out(AUX_B[14:8]), .DMC_Addr(dpcm_dmc_addr));
  TRIANGLE tria (
    .PHI1(PHI1), .n_ACLK(n_ACLK), .RES(RES), .W4008(RegOps[7]), .W400A(RegOps[8]), .W400B(RegOps[9]),
    .W401A(RegOps[16]), .n_LFO1(n_LFO1), .NOTRI(lc_notri), .LOCK(LOCK), .DB_in(D_In), .TRI_LC(tria_tri_lc),
    .TRI_Out(AUX_B[3:0]));
  DMA oam_dma (
    .ACLK(ACLK), .n_ACLK(n_ACLK), .PHI1(PHI1), .PHI2(PHI2), .RES(RES), .RnW(CPU_RnW), .W4014(RegOps[14]),
    .Dx_In(D_In), .RUNDMC(dpcm_rundmc), .n_DMC_AB(dpcm_n_dmcab), .DMCRDY(dpcm_dmcrdy),
    .DMC_Addr(dpcm_dmc_addr), .CPU_Addr(CPU_Ax), .Ax(APU_Ax), .Dx_Out(D_Out), .RW(APU_RW), .RDY(RDY));
  NOISE rnd (
    .ACLK(ACLK), .n_ACLK(n_ACLK), .RES(RES), .W400C(RegOps[20]), .W400E(RegOps[10]), .W400F(RegOps[24]),
    .n_LFO1(n_LFO1), .NORND(lc_nornd), .LOCK(LOCK), .DB_in(D_In), .RND_LC(rnd_rnd_lc), .RND_Out(AUX_B[7:4]));

  // Other names for the same wires on the sheet: n_R4018 = RegOps[0]; n_R401A = RegOps[1]; n_R4015 = RegOps[2];
  //   W4002 = RegOps[3]; W4001 = RegOps[4]; W4005 = RegOps[5]; W4006 = RegOps[6]; W4008 = RegOps[7];
  //   W400A = RegOps[8]; W400B = RegOps[9]; W400E = RegOps[10]; W4013 = RegOps[11]; W4012 = RegOps[12];
  //   W4010 = RegOps[13]; W4014 = RegOps[14]; n_R4019 = RegOps[15]; W401A = RegOps[16]; W4003 = RegOps[17];
  //   W4007 = RegOps[18]; W4004 = RegOps[19]; W400C = RegOps[20]; W4000 = RegOps[21]; W4015 = RegOps[22];
  //   W4011 = RegOps[23]; W400F = RegOps[24]; n_R4017 = RegOps[25]; n_R4016 = RegOps[26]; W4016 = RegOps[27];
  //   W4017 = RegOps[28]
endmodule

module DIV (
  input  n_CLK,
  input  PHI2,
  output PHI0,
  output n_M2
);

  wire not_1_out, not_2_out, not_3_out, nq, q, rst, SR0_nval, SR0_sout, SR1_nval, SR1_sout, SR2_nval,
       SR2_sout, SR3_nval, SR3_sout, SR4_nval, SR4_sout, SR5_nval, SR5_sout;

  not not_1 (not_1_out, n_CLK);
  not not_2 (not_2_out, not_1_out);
  nor nor_1 (nq, not_1_out, q);
  nor nor_2 (q, nq, not_2_out);
  // NoConnect on SR0_nval
  DIV_SRBit SR0 (.q(q), .nq(nq), .rst(rst), .sin(not_3_out), .nval(SR0_nval), .sout(SR0_sout));
  // NoConnect on SR3_nval
  DIV_SRBit SR3 (.q(q), .nq(nq), .rst(rst), .sin(SR2_sout), .nval(SR3_nval), .sout(SR3_sout));
  // NoConnect on SR1_nval
  DIV_SRBit SR1 (.q(q), .nq(nq), .rst(rst), .sin(SR0_sout), .nval(SR1_nval), .sout(SR1_sout));
  DIV_SRBit SR4 (.q(q), .nq(nq), .rst(1'b0), .sin(SR3_sout), .nval(SR4_nval), .sout(SR4_sout));
  DIV_SRBit SR2 (.q(q), .nq(nq), .rst(rst), .sin(SR1_sout), .nval(SR2_nval), .sout(SR2_sout));
  DIV_SRBit SR5 (.q(q), .nq(nq), .rst(1'b0), .sin(SR4_sout), .nval(SR5_nval), .sout(SR5_sout));
  // NoConnect on SR2_nval
  // NoConnect on SR5_nval
  not not_3 (not_3_out, SR5_sout);
  buf buffer_1 (PHI0, not_3_out);
  nor nor_3 (n_M2, SR4_nval, PHI2);
  nor nor_4 (rst, not_3_out, SR4_sout);

  // Notes on the sheet:
  //   Phase splitter
  //   CLK_FF
endmodule

module DIV_SRBit (
  input  q,
  input  nq,
  input  rst,
  input  sin,
  output nval,
  output sout
);

  wire out_latch_valout;

  DLatch in_latch (.Enable(q), .Value(sin), .n_ValOut(nval));  // open: ValOut
  DLatch out_latch (.Enable(nq), .Value(nval), .ValOut(out_latch_valout));  // open: n_ValOut
  nor nor_1 (sout, out_latch_valout, rst);
endmodule

module SoftCLK (
  input  PHI1,
  input  PHI2,
  input  RES,
  input  DMCINT,
  input  n_R4015,
  input  W4017,
  input  [7:0] D_In,
  output ACLK,
  output n_ACLK,
  output n_LFO1,
  output n_LFO2,
  output INT,
  output [7:0] D_Out
);

  wire and_1_out, control_f1_reset, control_f2_step, control_mode, nor_1_out, nor_2_out;
  wire [5:0] pla_pla;
  wire [14:0] sr15_n_sout, sr15_sout;

  ACLKGen aclk_gen (.PHI1(PHI1), .PHI2(PHI2), .RES(RES), .ACLK(ACLK), .n_ACLK(n_ACLK));
  SoftCLK_Control control (
    .n_ACLK(n_ACLK), .ACLK(ACLK), .PHI1(PHI1), .RES(RES), .pla(pla_pla), .DMCINT(DMCINT), .n_R4015(n_R4015),
    .W4017(W4017), .D_In(D_In), .mode(control_mode), .F1_Reset(control_f1_reset), .F2_Step(control_f2_step),
    .INT(INT), .n_LFO1(n_LFO1), .n_LFO2(n_LFO2), .D_Out(D_Out));
  and and_1 (and_1_out, sr15_sout[13], sr15_sout[14]);
  nor nor_1 (nor_1_out, and_1_out, nor_2_out);
  nor nor_2 (nor_2_out, sr15_sout[13], sr15_sout[14], pla_pla[5]);
  SoftCLK_SR sr15 (
    .n_ACLK(n_ACLK), .F1_Res(control_f1_reset), .F2_Step(control_f2_step), .sin(nor_1_out),
    .n_sout(sr15_n_sout), .sout(sr15_sout));
  SoftCLK_PLA pla (.ns(sr15_n_sout), .s(sr15_sout), .mode(control_mode), .pla(pla_pla));

  // Notes on the sheet:
  //   LFSR feedback
endmodule

module ACLKGen (
  input  PHI1,
  input  PHI2,
  input  RES,
  output ACLK,
  output n_ACLK
);

  wire nor_1_out, nor_2_out, nor_3_out, not_1_out, phi1_latch_n_valout, phi2_latch_n_valout;

  DLatch phi1_latch (.Enable(PHI1), .Value(nor_3_out), .n_ValOut(phi1_latch_n_valout));  // open: ValOut
  DLatch phi2_latch (.Enable(PHI2), .Value(phi1_latch_n_valout), .n_ValOut(phi2_latch_n_valout));  // open: ValOut
  not not_1 (not_1_out, PHI1);
  nor nor_1 (nor_1_out, not_1_out, nor_3_out);
  nor nor_2 (nor_2_out, not_1_out, phi2_latch_n_valout);
  nor nor_3 (nor_3_out, RES, phi2_latch_n_valout);
  not not_2 (ACLK, nor_1_out);
  buf buffer_1 (n_ACLK, nor_2_out);
endmodule

module SoftCLK_SR (
  input  n_ACLK,
  input  F1_Res,
  input  F2_Step,
  input  sin,
  output [14:0] n_sout,
  output [14:0] sout
);

  SoftCLK_SRBit softclk_srbit_1 (
    .n_ACLK(n_ACLK), .Res(F1_Res), .F2(F2_Step), .sin(sin), .n_sout(n_sout[0]), .sout(sout[0]));
  SoftCLK_SRBit softclk_srbit_2 (
    .n_ACLK(n_ACLK), .Res(F1_Res), .F2(F2_Step), .sin(sout[0]), .n_sout(n_sout[1]), .sout(sout[1]));
  SoftCLK_SRBit softclk_srbit_3 (
    .n_ACLK(n_ACLK), .Res(F1_Res), .F2(F2_Step), .sin(sout[1]), .n_sout(n_sout[2]), .sout(sout[2]));
  SoftCLK_SRBit softclk_srbit_4 (
    .n_ACLK(n_ACLK), .Res(F1_Res), .F2(F2_Step), .sin(sout[2]), .n_sout(n_sout[3]), .sout(sout[3]));
  SoftCLK_SRBit softclk_srbit_5 (
    .n_ACLK(n_ACLK), .Res(F1_Res), .F2(F2_Step), .sin(sout[3]), .n_sout(n_sout[4]), .sout(sout[4]));
  SoftCLK_SRBit softclk_srbit_6 (
    .n_ACLK(n_ACLK), .Res(F1_Res), .F2(F2_Step), .sin(sout[4]), .n_sout(n_sout[5]), .sout(sout[5]));
  SoftCLK_SRBit softclk_srbit_7 (
    .n_ACLK(n_ACLK), .Res(F1_Res), .F2(F2_Step), .sin(sout[5]), .n_sout(n_sout[6]), .sout(sout[6]));
  SoftCLK_SRBit softclk_srbit_8 (
    .n_ACLK(n_ACLK), .Res(F1_Res), .F2(F2_Step), .sin(sout[6]), .n_sout(n_sout[7]), .sout(sout[7]));
  SoftCLK_SRBit softclk_srbit_9 (
    .n_ACLK(n_ACLK), .Res(F1_Res), .F2(F2_Step), .sin(sout[7]), .n_sout(n_sout[8]), .sout(sout[8]));
  SoftCLK_SRBit softclk_srbit_10 (
    .n_ACLK(n_ACLK), .Res(F1_Res), .F2(F2_Step), .sin(sout[8]), .n_sout(n_sout[9]), .sout(sout[9]));
  SoftCLK_SRBit softclk_srbit_11 (
    .n_ACLK(n_ACLK), .Res(F1_Res), .F2(F2_Step), .sin(sout[9]), .n_sout(n_sout[10]), .sout(sout[10]));
  SoftCLK_SRBit softclk_srbit_12 (
    .n_ACLK(n_ACLK), .Res(F1_Res), .F2(F2_Step), .sin(sout[10]), .n_sout(n_sout[11]), .sout(sout[11]));
  SoftCLK_SRBit softclk_srbit_13 (
    .n_ACLK(n_ACLK), .Res(F1_Res), .F2(F2_Step), .sin(sout[11]), .n_sout(n_sout[12]), .sout(sout[12]));
  SoftCLK_SRBit softclk_srbit_14 (
    .n_ACLK(n_ACLK), .Res(F1_Res), .F2(F2_Step), .sin(sout[12]), .n_sout(n_sout[13]), .sout(sout[13]));
  SoftCLK_SRBit softclk_srbit_15 (
    .n_ACLK(n_ACLK), .Res(F1_Res), .F2(F2_Step), .sin(sout[13]), .n_sout(n_sout[14]), .sout(sout[14]));
endmodule

module SoftCLK_SRBit (
  input  n_ACLK,
  input  Res,
  input  F2,
  input  sin,
  output n_sout,
  output sout
);

  wire in_latch_nq, multiplexer_1_out, multiplexer_2_out, undriven;

  // NoConnect on undriven
  Multiplexer multiplexer_1 (.in0(undriven), .in1(1'b1), .out(multiplexer_1_out), .sel(Res));
  Multiplexer multiplexer_2 (.in0(multiplexer_1_out), .in1(sin), .out(multiplexer_2_out), .sel(F2));
  TranspDLatch in_latch (.d(multiplexer_2_out), .nq(in_latch_nq));  // open: q
  DLatch out_latch (.Enable(n_ACLK), .Value(in_latch_nq), .ValOut(n_sout), .n_ValOut(sout));
endmodule

module SoftCLK_PLA (
  input  [14:0] ns,
  input  [14:0] s,
  input  mode,
  output [5:0] pla
);

  nor nor_1 (pla[0], ns[0], s[1], s[2], s[3], s[4], ns[5], ns[6], s[7], s[8], s[9], s[10], s[11], ns[12], s[13], s[14]);
  nor nor_2 (pla[1], ns[0], ns[1], s[2], s[3], s[4], s[5], s[6], s[7], s[8], ns[9], ns[10], s[11], ns[12], ns[13], s[14]);
  nor nor_3 (pla[2], ns[0], ns[1], s[2], s[3], ns[4], s[5], ns[6], ns[7], s[8], s[9], ns[10], ns[11], s[12], ns[13], s[14]);
  nor nor_4 (pla[3], ns[0], ns[1], ns[2], ns[3], ns[4], s[5], s[6], s[7], s[8], ns[9], s[10], ns[11], s[12], s[13], s[14], mode);
  nor nor_5 (pla[4], ns[0], s[1], ns[2], s[3], s[4], s[5], s[6], ns[7], ns[8], s[9], s[10], s[11], ns[12], ns[13], ns[14]);
  nor nor_6 (pla[5], s[0], s[1], s[2], s[3], s[4], s[5], s[6], s[7], s[8], s[9], s[10], s[11], s[12], s[13], s[14]);

  // Notes on the sheet:
  //   nor-16
endmodule

module SoftCLK_Control (
  input  n_ACLK,
  input  ACLK,
  input  PHI1,
  input  RES,
  input  [5:0] pla,
  input  DMCINT,
  input  n_R4015,
  input  W4017,
  input  [7:0] D_In,
  output mode,
  output F1_Reset,
  output F2_Step,
  output INT,
  output n_LFO1,
  output n_LFO2,
  output [7:0] D_Out
);

  wire and_1_out, int_status_n_valout, int_status_valout, md_latch_valout, n_md, nor_1_out, nor_2_out,
       nor_3_out, nor_4_out, nor_5_out, nor_7_out, nor_8_out, nor_10_out, nor_11_out, nor_12_out, nor_13_out,
       nor_15_out, not_3_out, not_4_out, reg_mask_valout, Z1, z1_valout, Z2, z2_valout;

  // NoConnect on pla[5]
  nor nor_1 (nor_1_out, pla[0], pla[1], pla[2], pla[3], pla[4], Z2);
  nor nor_2 (nor_2_out, pla[1], pla[3], pla[4], Z2);
  nor nor_3 (nor_3_out, nor_1_out, ACLK);
  nor nor_4 (nor_4_out, nor_2_out, ACLK);
  RegisterBit reg_mode (.n_ACLK(n_ACLK), .Enable(W4017), .Value(D_In[7]), .n_ValOut(n_md));  // open: ValOut
  RegisterBit reg_mask (.n_ACLK(n_ACLK), .Enable(W4017), .Value(D_In[6]), .ValOut(reg_mask_valout));  // open: n_ValOut
  nor nor_5 (nor_5_out, Z1, pla[3], pla[4]);
  not not_1 (n_LFO1, nor_3_out);
  not not_2 (n_LFO2, nor_4_out);
  DLatch md_latch (.Enable(n_ACLK), .Value(n_md), .ValOut(md_latch_valout), .n_ValOut(mode));
  not not_3 (not_3_out, nor_5_out);
  nor nor_6 (F1_Reset, nor_5_out, ACLK);
  nor nor_7 (nor_7_out, z1_valout, ACLK);
  // NoConnect on md_latch_valout
  and and_1 (and_1_out, n_md, pla[3]);
  nor nor_8 (nor_8_out, n_R4015, PHI1);
  nor nor_9 (F2_Step, ACLK, not_3_out);
  DLatch u_z2 (.Enable(n_ACLK), .Value(n_md), .ValOut(z2_valout));  // open: n_ValOut
  nor nor_10 (nor_10_out, nor_7_out, nor_11_out);
  nor nor_11 (nor_11_out, nor_10_out, W4017, RES);
  nor nor_12 (nor_12_out, and_1_out, nor_13_out);
  nor nor_13 (nor_13_out, nor_12_out, nor_8_out, reg_mask_valout, RES);
  DLatch u_z1 (.Enable(n_ACLK), .Value(nor_11_out), .ValOut(z1_valout), .n_ValOut(Z1));
  DLatch int_status (.Enable(n_ACLK), .Value(nor_12_out), .ValOut(int_status_valout), .n_ValOut(int_status_n_valout));
  nor nor_14 (Z2, z2_valout, z1_valout);
  not not_4 (not_4_out, n_R4015);
  assign D_Out[6] = not_4_out ? ~int_status_valout : 1'bz;  // Controlled_Inverter controlled_inverter_1
  // NoConnect on int_status_n_valout
  nor nor_15 (nor_15_out, nor_13_out, DMCINT);
  not not_5 (INT, nor_15_out);

  // Notes on the sheet:
  //   LFO Outputs
  //   z_ff
  //   mode to PLA
  //   int_ff
  //   LFSR operation
  //   LFSR reload
  //   self-clear FF
  //   to core
endmodule

module RWDecode (
  input  APU_RW,
  input  n_R4015,
  input  DBG,
  input  n_REGRD,
  output WR,
  output RD
);

  wire nand_1_out, nand_2_out, not_1_out, not_2_out;

  not not_1 (not_1_out, n_REGRD);
  nand nand_1 (nand_1_out, DBG, not_1_out);
  nand nand_2 (nand_2_out, n_R4015, APU_RW, nand_1_out);
  buf buffer_1 (WR, nand_2_out);
  not not_2 (not_2_out, APU_RW);
  not not_3 (RD, not_2_out);

  // Notes on the sheet:
  //   from DMA buf
endmodule

module RegPredecode (
  input  [15:0] CPU_Ax,
  input  CPU_RnW,
  output n_REGRD,
  output n_REGWR
);

  wire nor_1_out, nor_2_out, not_1_out, not_2_out, not_3_out;

  not not_1 (not_1_out, CPU_Ax[14]);
  not not_2 (not_2_out, CPU_Ax[14]);
  not not_3 (not_3_out, CPU_RnW);
  nor nor_1 (nor_1_out, CPU_Ax[5], CPU_Ax[6], CPU_Ax[7], CPU_Ax[8], CPU_Ax[9], CPU_Ax[10], CPU_Ax[11], CPU_Ax[12], CPU_Ax[13], not_1_out, CPU_Ax[15], not_3_out);
  not not_4 (n_REGRD, nor_1_out);
  nor nor_2 (nor_2_out, CPU_Ax[5], CPU_Ax[6], CPU_Ax[7], CPU_Ax[8], CPU_Ax[9], CPU_Ax[10], CPU_Ax[11], CPU_Ax[12], CPU_Ax[13], not_2_out, CPU_Ax[15], CPU_RnW);
  not not_5 (n_REGWR, nor_2_out);

  // Notes on the sheet:
  //   nor 12
  //   nor 12
endmodule

module RegSel (
  input  PHI1,
  input  DBG,
  input  n_REGRD,
  input  n_REGWR,
  input  [15:0] APU_Ax,
  output n_R4018,
  output n_R401A,
  output n_R4015,
  output W4002,
  output W4001,
  output W4005,
  output W4006,
  output W4008,
  output W400A,
  output W400B,
  output W400E,
  output W4013,
  output W4012,
  output W4010,
  output W4014,
  output n_R4019,
  output W401A,
  output W4003,
  output W4007,
  output W4004,
  output W400C,
  output W4000,
  output W4015,
  output W4011,
  output W400F,
  output n_R4017,
  output n_R4016,
  output W4016,
  output W4017
);

  wire nand_4_out, nor_1_out, nor_2_out, nor_3_out, nor_4_out, nor_5_out, nor_6_out, nor_7_out, nor_8_out,
       nor_9_out, nor_10_out, nor_11_out, nor_12_out, nor_13_out, nor_14_out, nor_15_out, nor_28_out,
       nor_29_out, nor_30_out, nor_31_out, nor_32_out, nor_33_out, nor_34_out, nor_35_out, nor_36_out,
       nor_37_out, nor_38_out, nor_39_out, nor_40_out, nor_41_out, not_3_out, not_4_out, not_5_out,
       not_6_out, not_7_out, not_8_out, not_9_out, not_10_out, not_11_out, not_12_out, not_13_out,
       not_14_out, not_15_out, not_16_out, not_17_out, not_18_out, not_19_out, not_20_out, not_21_out,
       not_22_out, not_25_out, not_26_out;
  wire [4:0] not_1_out;

  // NoConnect on APU_Ax[5]
  // NoConnect on APU_Ax[6]
  // NoConnect on APU_Ax[7]
  // NoConnect on APU_Ax[8]
  // NoConnect on APU_Ax[9]
  // NoConnect on APU_Ax[10]
  // NoConnect on APU_Ax[11]
  // NoConnect on APU_Ax[12]
  // NoConnect on APU_Ax[13]
  // NoConnect on APU_Ax[14]
  // NoConnect on APU_Ax[15]
  assign not_1_out = ~APU_Ax[4:0];  // NOT_Gate not_1, 5 bits wide
  nor nor_1 (nor_1_out, APU_Ax[0], APU_Ax[1], APU_Ax[2], not_1_out[3], not_1_out[4], n_REGRD);
  nor nor_2 (nor_2_out, APU_Ax[0], not_1_out[1], APU_Ax[2], not_1_out[3], not_1_out[4], n_REGRD);
  nor nor_3 (nor_3_out, not_1_out[0], APU_Ax[1], not_1_out[2], APU_Ax[3], not_1_out[4], n_REGRD);
  nor nor_4 (nor_4_out, APU_Ax[0], not_1_out[1], APU_Ax[2], APU_Ax[3], APU_Ax[4], n_REGWR);
  nor nor_5 (nor_5_out, not_1_out[0], APU_Ax[1], APU_Ax[2], APU_Ax[3], APU_Ax[4], n_REGWR);
  nor nor_6 (nor_6_out, not_1_out[0], APU_Ax[1], not_1_out[2], APU_Ax[3], APU_Ax[4], n_REGWR);
  nor nor_7 (nor_7_out, APU_Ax[0], not_1_out[1], not_1_out[2], APU_Ax[3], APU_Ax[4], n_REGWR);
  nor nor_8 (nor_8_out, APU_Ax[0], APU_Ax[1], APU_Ax[2], not_1_out[3], APU_Ax[4], n_REGWR);
  nor nor_9 (nor_9_out, APU_Ax[0], not_1_out[1], APU_Ax[2], not_1_out[3], APU_Ax[4], n_REGWR);
  nor nor_10 (nor_10_out, not_1_out[0], not_1_out[1], APU_Ax[2], not_1_out[3], APU_Ax[4], n_REGWR);
  nor nor_11 (nor_11_out, APU_Ax[0], not_1_out[1], not_1_out[2], not_1_out[3], APU_Ax[4], n_REGWR);
  nor nor_12 (nor_12_out, not_1_out[0], not_1_out[1], APU_Ax[2], APU_Ax[3], not_1_out[4], n_REGWR);
  nor nor_13 (nor_13_out, APU_Ax[0], not_1_out[1], APU_Ax[2], APU_Ax[3], not_1_out[4], n_REGWR);
  nor nor_14 (nor_14_out, APU_Ax[0], APU_Ax[1], APU_Ax[2], APU_Ax[3], not_1_out[4], n_REGWR);
  nor nor_15 (nor_15_out, APU_Ax[0], APU_Ax[1], not_1_out[2], APU_Ax[3], not_1_out[4], n_REGWR);
  not not_2 (n_R4015, nor_3_out);
  not not_3 (not_3_out, nor_4_out);
  not not_4 (not_4_out, nor_5_out);
  not not_5 (not_5_out, nor_6_out);
  not not_6 (not_6_out, nor_7_out);
  not not_7 (not_7_out, nor_8_out);
  not not_8 (not_8_out, nor_9_out);
  not not_9 (not_9_out, nor_10_out);
  not not_10 (not_10_out, nor_11_out);
  not not_11 (not_11_out, nor_12_out);
  not not_12 (not_12_out, nor_13_out);
  not not_13 (not_13_out, nor_14_out);
  not not_14 (not_14_out, nor_15_out);
  nand nand_1 (n_R4018, DBG, nor_1_out);
  nand nand_2 (n_R401A, DBG, nor_2_out);
  nor nor_16 (W4002, PHI1, not_3_out);
  nor nor_17 (W4001, PHI1, not_4_out);
  nor nor_18 (W4005, PHI1, not_5_out);
  nor nor_19 (W4006, PHI1, not_6_out);
  nor nor_20 (W4008, PHI1, not_7_out);
  nor nor_21 (W400A, PHI1, not_8_out);
  nor nor_22 (W400B, PHI1, not_9_out);
  nor nor_23 (W400E, PHI1, not_10_out);
  nor nor_24 (W4013, PHI1, not_11_out);
  nor nor_25 (W4012, PHI1, not_12_out);
  nor nor_26 (W4010, PHI1, not_13_out);
  nor nor_27 (W4014, PHI1, not_14_out);
  nor nor_28 (nor_28_out, not_1_out[0], APU_Ax[1], APU_Ax[2], not_1_out[3], not_1_out[4], n_REGRD);
  nor nor_29 (nor_29_out, APU_Ax[0], not_1_out[1], APU_Ax[2], not_1_out[3], not_1_out[4], n_REGWR);
  nor nor_30 (nor_30_out, not_1_out[0], not_1_out[1], APU_Ax[2], APU_Ax[3], APU_Ax[4], n_REGWR);
  not not_15 (not_15_out, nor_30_out);
  nor nor_31 (nor_31_out, not_1_out[0], not_1_out[1], not_1_out[2], APU_Ax[3], APU_Ax[4], n_REGWR);
  not not_16 (not_16_out, nor_31_out);
  nor nor_32 (nor_32_out, APU_Ax[0], APU_Ax[1], not_1_out[2], APU_Ax[3], APU_Ax[4], n_REGWR);
  not not_17 (not_17_out, nor_32_out);
  nor nor_33 (nor_33_out, APU_Ax[0], APU_Ax[1], not_1_out[2], not_1_out[3], APU_Ax[4], n_REGWR);
  not not_18 (not_18_out, nor_33_out);
  nor nor_34 (nor_34_out, APU_Ax[0], APU_Ax[1], APU_Ax[2], APU_Ax[3], APU_Ax[4], n_REGWR);
  not not_19 (not_19_out, nor_34_out);
  nor nor_35 (nor_35_out, not_1_out[0], APU_Ax[1], not_1_out[2], APU_Ax[3], not_1_out[4], n_REGWR);
  not not_20 (not_20_out, nor_35_out);
  nor nor_36 (nor_36_out, not_1_out[0], APU_Ax[1], APU_Ax[2], APU_Ax[3], not_1_out[4], n_REGWR);
  not not_21 (not_21_out, nor_36_out);
  nor nor_37 (nor_37_out, not_1_out[0], not_1_out[1], not_1_out[2], not_1_out[3], APU_Ax[4], n_REGWR);
  not not_22 (not_22_out, nor_37_out);
  nor nor_38 (nor_38_out, not_1_out[0], not_1_out[1], not_1_out[2], APU_Ax[3], not_1_out[4], n_REGRD);
  not not_23 (n_R4017, nor_38_out);
  nor nor_39 (nor_39_out, APU_Ax[0], not_1_out[1], not_1_out[2], APU_Ax[3], not_1_out[4], n_REGRD);
  not not_24 (n_R4016, nor_39_out);
  nor nor_40 (nor_40_out, APU_Ax[0], not_1_out[1], not_1_out[2], APU_Ax[3], not_1_out[4], n_REGWR);
  not not_25 (not_25_out, nor_40_out);
  nor nor_41 (nor_41_out, not_1_out[0], not_1_out[1], not_1_out[2], APU_Ax[3], not_1_out[4], n_REGWR);
  not not_26 (not_26_out, nor_41_out);
  nand nand_3 (n_R4019, DBG, nor_28_out);
  nand nand_4 (nand_4_out, DBG, nor_29_out);
  nor nor_42 (W4003, PHI1, not_15_out);
  nor nor_43 (W4007, PHI1, not_16_out);
  nor nor_44 (W4004, PHI1, not_17_out);
  nor nor_45 (W400C, PHI1, not_18_out);
  nor nor_46 (W4000, PHI1, not_19_out);
  nor nor_47 (W4015, PHI1, not_20_out);
  nor nor_48 (W4011, PHI1, not_21_out);
  nor nor_49 (W400F, PHI1, not_22_out);
  nor nor_50 (W4016, PHI1, not_25_out);
  nor nor_51 (W4017, PHI1, not_26_out);
  nor nor_52 (W401A, PHI1, nand_4_out);

  // Notes on the sheet:
  //   address complement
endmodule

module DebugLock (
  input  W401A,
  input  n_ACLK,
  input  RES,
  input  [7:0] D_In,
  output APU_LOCK
);

  wire lock_latch_nq, multiplexer_1_out, multiplexer_2_out, undriven;

  // NoConnect on undriven
  Multiplexer multiplexer_1 (.in0(undriven), .in1(D_In[7]), .out(multiplexer_1_out), .sel(W401A));
  Multiplexer multiplexer_2 (.in0(multiplexer_1_out), .in1(APU_LOCK), .out(multiplexer_2_out), .sel(n_ACLK));
  nor nor_1 (APU_LOCK, lock_latch_nq, RES);
  TranspDLatch lock_latch (.d(multiplexer_2_out), .nq(lock_latch_nq));  // open: q
endmodule

module OUT_Ports (
  input  W4016,
  input  ACLK,
  input  n_ACLK,
  input  [7:0] D_In,
  output OUT_0,
  output OUT_1,
  output OUT_2
);

  wire nACLK5;

  not not_1 (nACLK5, ACLK);
  IORegBit out0 (.W4016(W4016), .Other_nACLK(nACLK5), .n_ACLK(n_ACLK), .D_x(D_In[0]), .OUT_x(OUT_0));
  IORegBit out1 (.W4016(W4016), .Other_nACLK(nACLK5), .n_ACLK(n_ACLK), .D_x(D_In[1]), .OUT_x(OUT_1));
  IORegBit out2 (.W4016(W4016), .Other_nACLK(nACLK5), .n_ACLK(n_ACLK), .D_x(D_In[2]), .OUT_x(OUT_2));
endmodule

module IORegBit (
  input  W4016,
  input  Other_nACLK,
  input  n_ACLK,
  input  D_x,
  output OUT_x
);

  wire dlatch_1_n_valout, multiplexer_1_out, multiplexer_2_out, not_1_out, transpdlatch_1_nq, undriven;

  // NoConnect on undriven
  Multiplexer multiplexer_1 (.in0(undriven), .in1(D_x), .out(multiplexer_1_out), .sel(W4016));
  Multiplexer multiplexer_2 (.in0(multiplexer_1_out), .in1(not_1_out), .out(multiplexer_2_out), .sel(n_ACLK));
  not not_1 (not_1_out, transpdlatch_1_nq);
  DLatch dlatch_1 (.Enable(Other_nACLK), .Value(not_1_out), .n_ValOut(dlatch_1_n_valout));  // open: ValOut
  TranspDLatch transpdlatch_1 (.d(multiplexer_2_out), .nq(transpdlatch_1_nq));  // open: q
  not not_2 (OUT_x, dlatch_1_n_valout);
endmodule

module TranspDLatch (
  input  d,
  output q,
  output nq
);

  D_Flip_Flop #(.trigger("high")) d_ff_1 (.D(d), .clk(1'b1), .Q(q), .Qn(nq));  // open: preset, reset
endmodule

module BIDIR_Pad (
  input  pad_in,
  input  to_pad,
  input  rd,
  input  wr,
  output from_pad,
  output pad_out
);

  wire nor_1_out, not_1_out, not_2_out, not_3_out, not_4_out, transpdlatch_1_nq, transpdlatch_2_q;

  Transistor #(.\type ("n")) transistor_1 (.in(1'b0), .out(pad_in), .gate(1'b0));
  TranspDLatch transpdlatch_1 (.d(pad_in), .nq(transpdlatch_1_nq));  // open: q
  TranspDLatch transpdlatch_2 (.d(to_pad), .q(transpdlatch_2_q));  // open: nq
  not not_1 (not_1_out, wr);
  not not_2 (not_2_out, transpdlatch_1_nq);
  not not_3 (not_3_out, not_2_out);
  not not_4 (not_4_out, rd);
  nor nor_1 (nor_1_out, transpdlatch_2_q, rd);
  assign from_pad = not_1_out ? ~not_3_out : 1'bz;  // Controlled_Inverter controlled_inverter_1
  assign pad_out = not_4_out ? ~nor_1_out : 1'bz;  // Controlled_Inverter controlled_inverter_2

  // Notes on the sheet:
  //   ESD
endmodule

module Pads1 (
  input  CLK_Pad,
  input  DBG_Pad,
  input  n_M2,
  input  n_RES_Pad,
  input  Ax,
  input  RW,
  output M2_Pad,
  output Ax_Pad,
  output RnW_Pad
);

  wire n_CLK, nor_1_out, nor_2_out, nor_4_out, not_1_out, not_2_out, not_3_out, not_4_out, not_6_out,
       not_7_out, not_8_out, not_9_out, not_10_out, not_11_out, not_13_out, not_14_out, not_15_out,
       not_16_out, not_17_out, not_18_out, not_19_out, not_20_out, not_21_out, not_22_out, NotDBG_RES, RES;

  Transistor #(.\type ("n")) transistor_1 (.in(1'b0), .out(CLK_Pad), .gate(1'b0));
  Transistor #(.\type ("n")) transistor_2 (.in(1'b0), .out(DBG_Pad), .gate(1'b0));
  Transistor #(.\type ("n")) transistor_3 (.in(1'b0), .out(n_RES_Pad), .gate(1'b0));
  not not_1 (not_1_out, Ax);
  not not_2 (not_2_out, not_1_out);
  not not_3 (not_3_out, RW);
  not not_4 (not_4_out, not_3_out);
  not not_5 (n_CLK, CLK_Pad);
  Pull_Resistor #(.pull(1)) pull_resistor_1 (.node(n_RES_Pad));
  not not_6 (not_6_out, n_RES_Pad);
  not not_7 (not_7_out, not_2_out);
  not not_8 (not_8_out, not_7_out);
  not not_9 (not_9_out, not_4_out);
  not not_10 (not_10_out, not_9_out);
  not not_11 (not_11_out, not_6_out);
  not not_12 (RES, not_11_out);
  not not_13 (not_13_out, not_8_out);
  not not_14 (not_14_out, not_13_out);
  not not_15 (not_15_out, not_10_out);
  not not_16 (not_16_out, not_15_out);
  not not_17 (not_17_out, DBG_Pad);
  not not_18 (not_18_out, not_17_out);
  not not_19 (not_19_out, RES);
  not not_20 (not_20_out, RES);
  nor nor_1 (nor_1_out, not_14_out, RES);
  not not_21 (not_21_out, RES);
  nor nor_2 (nor_2_out, not_16_out, RES);
  nor nor_3 (NotDBG_RES, not_18_out, not_19_out);
  assign Ax_Pad = not_20_out ? ~nor_1_out : 1'bz;  // Controlled_Inverter controlled_inverter_1
  assign RnW_Pad = not_21_out ? ~nor_2_out : 1'bz;  // Controlled_Inverter controlled_inverter_2
  not not_22 (not_22_out, NotDBG_RES);
  nor nor_4 (nor_4_out, n_M2, NotDBG_RES);
  assign M2_Pad = not_22_out ? nor_4_out : 1'bz;  // Controlled_Buffer controlled_buffer_1

  // Other names for the same wires on the sheet: DBG = DBG_Pad

  // Notes on the sheet:
  //   ESD
  //   ESD
  //   ESD
  //   x6
  //   x6
  //   to div
endmodule

module Pads2 (
  input  n_IRQ_Pad,
  input  n_NMI_Pad,
  input  DPad_in,
  input  Dx_in,
  input  RD,
  input  WR,
  input  RES,
  input  n_R4016,
  input  n_R4017,
  input  OUTx,
  output Dx_out,
  output DPad_out,
  output n_IN0_Pad,
  output n_IN1_Pad,
  output OUT_Pad
);

  wire bidir_pad_1_pad_out, bidir_pad_2_pad_out, bidir_pad_4_from_pad, bidir_pad_5_from_pad,
       bidir_pad_6_from_pad, n_IRQ, n_NMI, undriven, undriven_2, undriven_3;

  // NoConnect on undriven
  // NoConnect on undriven_2
  // NoConnect on undriven_3
  BIDIR_Pad bidir_pad_1 (
    .pad_in(n_IRQ_Pad), .to_pad(1'b1), .rd(1'b1), .wr(1'b0), .from_pad(n_IRQ), .pad_out(bidir_pad_1_pad_out));
  // NoConnect on bidir_pad_1_pad_out
  BIDIR_Pad bidir_pad_2 (
    .pad_in(n_NMI_Pad), .to_pad(1'b1), .rd(1'b1), .wr(1'b0), .from_pad(n_NMI), .pad_out(bidir_pad_2_pad_out));
  // NoConnect on bidir_pad_2_pad_out
  BIDIR_Pad bidir_pad_3 (.pad_in(DPad_in), .to_pad(Dx_in), .rd(RD), .wr(WR), .from_pad(Dx_out), .pad_out(DPad_out));
  // NoConnect on bidir_pad_4_from_pad
  BIDIR_Pad bidir_pad_4 (
    .pad_in(undriven), .to_pad(n_R4016), .rd(RES), .wr(1'b1), .from_pad(bidir_pad_4_from_pad),
    .pad_out(n_IN0_Pad));
  // NoConnect on bidir_pad_5_from_pad
  BIDIR_Pad bidir_pad_5 (
    .pad_in(undriven_2), .to_pad(n_R4017), .rd(RES), .wr(1'b1), .from_pad(bidir_pad_5_from_pad),
    .pad_out(n_IN1_Pad));
  // NoConnect on bidir_pad_6_from_pad
  BIDIR_Pad bidir_pad_6 (
    .pad_in(undriven_3), .to_pad(OUTx), .rd(RES), .wr(1'b1), .from_pad(bidir_pad_6_from_pad),
    .pad_out(OUT_Pad));

  // Notes on the sheet:
  //   I/O
  //   Data bus
endmodule

module DataBusPads (
  input  [7:0] Pads_In,
  input  [7:0] DB_In,
  input  RD,
  input  WR,
  output [7:0] DB_Out,
  output [7:0] Pads_Out
);

  BIDIR_Pad bidir_pad_1 (
    .pad_in(Pads_In[0]), .to_pad(DB_In[0]), .rd(RD), .wr(WR), .from_pad(DB_Out[0]), .pad_out(Pads_Out[0]));
  BIDIR_Pad bidir_pad_2 (
    .pad_in(Pads_In[1]), .to_pad(DB_In[1]), .rd(RD), .wr(WR), .from_pad(DB_Out[1]), .pad_out(Pads_Out[1]));
  BIDIR_Pad bidir_pad_3 (
    .pad_in(Pads_In[2]), .to_pad(DB_In[2]), .rd(RD), .wr(WR), .from_pad(DB_Out[2]), .pad_out(Pads_Out[2]));
  BIDIR_Pad bidir_pad_4 (
    .pad_in(Pads_In[3]), .to_pad(DB_In[3]), .rd(RD), .wr(WR), .from_pad(DB_Out[3]), .pad_out(Pads_Out[3]));
  BIDIR_Pad bidir_pad_5 (
    .pad_in(Pads_In[4]), .to_pad(DB_In[4]), .rd(RD), .wr(WR), .from_pad(DB_Out[4]), .pad_out(Pads_Out[4]));
  BIDIR_Pad bidir_pad_6 (
    .pad_in(Pads_In[5]), .to_pad(DB_In[5]), .rd(RD), .wr(WR), .from_pad(DB_Out[5]), .pad_out(Pads_Out[5]));
  BIDIR_Pad bidir_pad_7 (
    .pad_in(Pads_In[6]), .to_pad(DB_In[6]), .rd(RD), .wr(WR), .from_pad(DB_Out[6]), .pad_out(Pads_Out[6]));
  BIDIR_Pad bidir_pad_8 (
    .pad_in(Pads_In[7]), .to_pad(DB_In[7]), .rd(RD), .wr(WR), .from_pad(DB_Out[7]), .pad_out(Pads_Out[7]));
endmodule

module DbgReadoutBit (
  input  n_rd,
  input  val,
  output Dx
);

  wire not_1_out;

  not not_1 (not_1_out, n_rd);
  assign Dx = not_1_out ? val : 1'bz;  // Controlled_Buffer controlled_buffer_1
endmodule

module Length_Decoder1 (
  input  [4:0] Dec1_In,
  output [31:0] Dec1_Out
);

  wire [4:0] not_1_out;

  assign not_1_out = ~Dec1_In;  // NOT_Gate not_1, 5 bits wide
  nor nor_1 (Dec1_Out[0], Dec1_In[0], Dec1_In[1], Dec1_In[2], Dec1_In[3], Dec1_In[4]);
  nor nor_2 (Dec1_Out[1], Dec1_In[0], not_1_out[1], Dec1_In[2], Dec1_In[3], Dec1_In[4]);
  nor nor_3 (Dec1_Out[2], Dec1_In[0], Dec1_In[1], not_1_out[2], Dec1_In[3], Dec1_In[4]);
  nor nor_4 (Dec1_Out[3], Dec1_In[0], not_1_out[1], not_1_out[2], Dec1_In[3], Dec1_In[4]);
  nor nor_5 (Dec1_Out[4], Dec1_In[0], Dec1_In[1], Dec1_In[2], not_1_out[3], Dec1_In[4]);
  nor nor_6 (Dec1_Out[5], Dec1_In[0], not_1_out[1], Dec1_In[2], not_1_out[3], Dec1_In[4]);
  nor nor_7 (Dec1_Out[6], Dec1_In[0], Dec1_In[1], not_1_out[2], not_1_out[3], Dec1_In[4]);
  nor nor_8 (Dec1_Out[7], Dec1_In[0], not_1_out[1], not_1_out[2], not_1_out[3], Dec1_In[4]);
  nor nor_9 (Dec1_Out[8], Dec1_In[0], Dec1_In[1], Dec1_In[2], Dec1_In[3], not_1_out[4]);
  nor nor_10 (Dec1_Out[9], Dec1_In[0], not_1_out[1], Dec1_In[2], Dec1_In[3], not_1_out[4]);
  nor nor_11 (Dec1_Out[10], Dec1_In[0], Dec1_In[1], not_1_out[2], Dec1_In[3], not_1_out[4]);
  nor nor_12 (Dec1_Out[11], Dec1_In[0], not_1_out[1], not_1_out[2], Dec1_In[3], not_1_out[4]);
  nor nor_13 (Dec1_Out[12], Dec1_In[0], Dec1_In[1], Dec1_In[2], not_1_out[3], not_1_out[4]);
  nor nor_14 (Dec1_Out[13], Dec1_In[0], not_1_out[1], Dec1_In[2], not_1_out[3], not_1_out[4]);
  nor nor_15 (Dec1_Out[14], Dec1_In[0], Dec1_In[1], not_1_out[2], not_1_out[3], not_1_out[4]);
  nor nor_16 (Dec1_Out[15], Dec1_In[0], not_1_out[1], not_1_out[2], not_1_out[3], not_1_out[4]);
  nor nor_17 (Dec1_Out[16], not_1_out[0], Dec1_In[1], Dec1_In[2], Dec1_In[3], Dec1_In[4]);
  nor nor_18 (Dec1_Out[17], not_1_out[0], not_1_out[1], Dec1_In[2], Dec1_In[3], Dec1_In[4]);
  nor nor_19 (Dec1_Out[18], not_1_out[0], Dec1_In[1], not_1_out[2], Dec1_In[3], Dec1_In[4]);
  nor nor_20 (Dec1_Out[19], not_1_out[0], not_1_out[1], not_1_out[2], Dec1_In[3], Dec1_In[4]);
  nor nor_21 (Dec1_Out[20], not_1_out[0], Dec1_In[1], Dec1_In[2], not_1_out[3], Dec1_In[4]);
  nor nor_22 (Dec1_Out[21], not_1_out[0], not_1_out[1], Dec1_In[2], not_1_out[3], Dec1_In[4]);
  nor nor_23 (Dec1_Out[22], not_1_out[0], Dec1_In[1], not_1_out[2], not_1_out[3], Dec1_In[4]);
  nor nor_24 (Dec1_Out[23], not_1_out[0], not_1_out[1], not_1_out[2], not_1_out[3], Dec1_In[4]);
  nor nor_25 (Dec1_Out[24], not_1_out[0], Dec1_In[1], Dec1_In[2], Dec1_In[3], not_1_out[4]);
  nor nor_26 (Dec1_Out[25], not_1_out[0], not_1_out[1], Dec1_In[2], Dec1_In[3], not_1_out[4]);
  nor nor_27 (Dec1_Out[26], not_1_out[0], Dec1_In[1], not_1_out[2], Dec1_In[3], not_1_out[4]);
  nor nor_28 (Dec1_Out[27], not_1_out[0], not_1_out[1], not_1_out[2], Dec1_In[3], not_1_out[4]);
  nor nor_29 (Dec1_Out[28], not_1_out[0], Dec1_In[1], Dec1_In[2], not_1_out[3], not_1_out[4]);
  nor nor_30 (Dec1_Out[29], not_1_out[0], not_1_out[1], Dec1_In[2], not_1_out[3], not_1_out[4]);
  nor nor_31 (Dec1_Out[30], not_1_out[0], Dec1_In[1], not_1_out[2], not_1_out[3], not_1_out[4]);
  nor nor_32 (Dec1_Out[31], not_1_out[0], not_1_out[1], not_1_out[2], not_1_out[3], not_1_out[4]);

  // Notes on the sheet:
  //   0
  //   2
  //   4
  //   6
  //   8
  //   10
  //   12
  //   14
  //   16
  //   18
  //   20
  //   22
  //   24
  //   26
  //   28
  //   30
  //   1
  //   3
  //   5
  //   7
  //   9
  //   11
  //   13
  //   15
  //   17
  //   19
  //   21
  //   23
  //   25
  //   27
  //   29
  //   31
endmodule

module Length_Decoder2 (
  input  [31:0] Dec2_In,
  output [7:0] Dec2_Out
);

  nor nor_1 (Dec2_Out[7], Dec2_In[0], Dec2_In[1], Dec2_In[2], Dec2_In[3], Dec2_In[5], Dec2_In[6], Dec2_In[7], Dec2_In[8], Dec2_In[9], Dec2_In[10], Dec2_In[11], Dec2_In[13], Dec2_In[14], Dec2_In[15], Dec2_In[17], Dec2_In[18], Dec2_In[19], Dec2_In[20], Dec2_In[21], Dec2_In[22], Dec2_In[23], Dec2_In[24], Dec2_In[25], Dec2_In[26], Dec2_In[27], Dec2_In[28], Dec2_In[29], Dec2_In[30], Dec2_In[31]);
  nor nor_2 (Dec2_Out[6], Dec2_In[0], Dec2_In[1], Dec2_In[2], Dec2_In[4], Dec2_In[5], Dec2_In[6], Dec2_In[7], Dec2_In[8], Dec2_In[9], Dec2_In[10], Dec2_In[12], Dec2_In[14], Dec2_In[15], Dec2_In[17], Dec2_In[18], Dec2_In[19], Dec2_In[20], Dec2_In[21], Dec2_In[22], Dec2_In[23], Dec2_In[24], Dec2_In[25], Dec2_In[26], Dec2_In[27], Dec2_In[28], Dec2_In[29], Dec2_In[30], Dec2_In[31]);
  nor nor_3 (Dec2_Out[5], Dec2_In[0], Dec2_In[1], Dec2_In[3], Dec2_In[4], Dec2_In[6], Dec2_In[7], Dec2_In[8], Dec2_In[9], Dec2_In[11], Dec2_In[13], Dec2_In[14], Dec2_In[15], Dec2_In[17], Dec2_In[18], Dec2_In[19], Dec2_In[20], Dec2_In[21], Dec2_In[22], Dec2_In[23], Dec2_In[24], Dec2_In[25], Dec2_In[26], Dec2_In[27], Dec2_In[28], Dec2_In[29], Dec2_In[30], Dec2_In[31]);
  nor nor_4 (Dec2_Out[4], Dec2_In[0], Dec2_In[2], Dec2_In[3], Dec2_In[6], Dec2_In[8], Dec2_In[10], Dec2_In[13], Dec2_In[14], Dec2_In[17], Dec2_In[18], Dec2_In[19], Dec2_In[20], Dec2_In[21], Dec2_In[22], Dec2_In[23], Dec2_In[24]);
  nor nor_5 (Dec2_Out[3], Dec2_In[1], Dec2_In[2], Dec2_In[9], Dec2_In[13], Dec2_In[17], Dec2_In[18], Dec2_In[19], Dec2_In[20], Dec2_In[25], Dec2_In[26], Dec2_In[27], Dec2_In[28]);
  nor nor_6 (Dec2_Out[2], Dec2_In[0], Dec2_In[1], Dec2_In[5], Dec2_In[7], Dec2_In[8], Dec2_In[17], Dec2_In[18], Dec2_In[21], Dec2_In[22], Dec2_In[25], Dec2_In[26], Dec2_In[29], Dec2_In[30]);
  nor nor_7 (Dec2_Out[1], Dec2_In[0], Dec2_In[6], Dec2_In[7], Dec2_In[16], Dec2_In[17], Dec2_In[19], Dec2_In[21], Dec2_In[23], Dec2_In[25], Dec2_In[27], Dec2_In[29], Dec2_In[31]);

  assign Dec2_Out[0] = 1'b1;

  // Notes on the sheet:
  //   7
  //   6
  //   5
  //   4
  //   3
  //   2
  //   1
endmodule

module Length_Decoder (
  input  [7:0] DB,
  output [7:0] LC
);

  wire [4:0] transpdlatch_1_q;
  wire [31:0] length_decoder1_1_dec1_out;

  TranspDLatch transpdlatch_1 (.d(DB[3]), .q(transpdlatch_1_q[0]));  // open: nq
  TranspDLatch transpdlatch_2 (.d(DB[4]), .q(transpdlatch_1_q[1]));  // open: nq
  TranspDLatch transpdlatch_3 (.d(DB[5]), .q(transpdlatch_1_q[2]));  // open: nq
  TranspDLatch transpdlatch_4 (.d(DB[6]), .q(transpdlatch_1_q[3]));  // open: nq
  TranspDLatch transpdlatch_5 (.d(DB[7]), .q(transpdlatch_1_q[4]));  // open: nq
  Length_Decoder1 length_decoder1_1 (.Dec1_In(transpdlatch_1_q), .Dec1_Out(length_decoder1_1_dec1_out));
  Length_Decoder2 length_decoder2_1 (.Dec2_In(length_decoder1_1_dec1_out), .Dec2_Out(LC));
endmodule

module Length_Control (
  input  ACLK,
  input  n_ACLK,
  input  RES,
  input  n_LFO2,
  input  W4015,
  input  WriteEn,
  input  n_R4015,
  input  DB_Bit_in,
  input  CarryOut,
  output NO_LC,
  output DB_Bit_out,
  output STEP
);

  wire and_1_out, and_2_out, controlled_buffer_1_out, cout_latch_n_valout, cout_latch_valout,
       ena_latch_n_valout, ena_latch_valout, n_ACLK4, nor_1_out, nor_2_out, not_2_out, not_4_out,
       step_latch_n_valout, step_latch_valout, transpdlatch_1_nq;

  not not_1 (n_ACLK4, ACLK);
  assign controlled_buffer_1_out = n_ACLK ? not_2_out : 1'bz;  // Controlled_Buffer controlled_buffer_1
  assign controlled_buffer_1_out = W4015 ? DB_Bit_in : 1'bz;  // Controlled_Buffer controlled_buffer_2
  assign controlled_buffer_1_out = RES ? 1'b0 : 1'bz;  // Controlled_Buffer controlled_buffer_3
  not not_2 (not_2_out, transpdlatch_1_nq);
  TranspDLatch transpdlatch_1 (.d(controlled_buffer_1_out), .nq(transpdlatch_1_nq));  // open: q
  DLatch ena_latch (
    .Enable(n_ACLK), .Value(transpdlatch_1_nq), .ValOut(ena_latch_valout), .n_ValOut(ena_latch_n_valout));
  DLatch cout_latch (.Enable(n_ACLK), .Value(CarryOut), .ValOut(cout_latch_valout), .n_ValOut(cout_latch_n_valout));
  // NoConnect on ena_latch_n_valout
  // NoConnect on cout_latch_n_valout
  and and_1 (and_1_out, n_ACLK4, ena_latch_valout);
  and and_2 (and_2_out, cout_latch_valout, STEP);
  DLatch step_latch (.Enable(n_ACLK), .Value(nor_2_out), .ValOut(step_latch_valout), .n_ValOut(step_latch_n_valout));
  nor nor_1 (nor_1_out, and_1_out, and_2_out, RES, nor_2_out);
  nor nor_2 (nor_2_out, nor_1_out, WriteEn);
  // NoConnect on step_latch_n_valout
  not not_3 (NO_LC, nor_1_out);
  nor nor_3 (STEP, step_latch_valout, n_LFO2);
  not not_4 (not_4_out, n_R4015);
  assign DB_Bit_out = not_4_out ? ~nor_2_out : 1'bz;  // Controlled_Inverter controlled_inverter_1

  // Notes on the sheet:
  //   reg_enable
  //   disable
  //   stat_ff
  //   notif0
endmodule

module Length_Counter (
  input  n_ACLK,
  input  STEP,
  input  RES,
  input  WriteEn,
  input  [7:0] LC,
  input  CarryIn,
  output CarryOut
);

  wire downcounterbit_1_carryout, downcounterbit_2_carryout, downcounterbit_3_carryout,
       downcounterbit_4_carryout, downcounterbit_5_carryout, downcounterbit_6_carryout,
       downcounterbit_7_carryout;

  DownCounterBit downcounterbit_1 (
    .n_ACLK(n_ACLK), .Load(WriteEn), .Value(LC[0]), .Clear(RES), .Step(STEP), .CarryIn(CarryIn),
    .CarryOut(downcounterbit_1_carryout));  // open: n_CntOut, CntOut
  DownCounterBit downcounterbit_2 (
    .n_ACLK(n_ACLK), .Load(WriteEn), .Value(LC[1]), .Clear(RES), .Step(STEP),
    .CarryIn(downcounterbit_1_carryout), .CarryOut(downcounterbit_2_carryout));  // open: n_CntOut, CntOut
  DownCounterBit downcounterbit_3 (
    .n_ACLK(n_ACLK), .Load(WriteEn), .Value(LC[2]), .Clear(RES), .Step(STEP),
    .CarryIn(downcounterbit_2_carryout), .CarryOut(downcounterbit_3_carryout));  // open: n_CntOut, CntOut
  DownCounterBit downcounterbit_4 (
    .n_ACLK(n_ACLK), .Load(WriteEn), .Value(LC[3]), .Clear(RES), .Step(STEP),
    .CarryIn(downcounterbit_3_carryout), .CarryOut(downcounterbit_4_carryout));  // open: n_CntOut, CntOut
  DownCounterBit downcounterbit_5 (
    .n_ACLK(n_ACLK), .Load(WriteEn), .Value(LC[4]), .Clear(RES), .Step(STEP),
    .CarryIn(downcounterbit_4_carryout), .CarryOut(downcounterbit_5_carryout));  // open: n_CntOut, CntOut
  DownCounterBit downcounterbit_6 (
    .n_ACLK(n_ACLK), .Load(WriteEn), .Value(LC[5]), .Clear(RES), .Step(STEP),
    .CarryIn(downcounterbit_5_carryout), .CarryOut(downcounterbit_6_carryout));  // open: n_CntOut, CntOut
  DownCounterBit downcounterbit_7 (
    .n_ACLK(n_ACLK), .Load(WriteEn), .Value(LC[6]), .Clear(RES), .Step(STEP),
    .CarryIn(downcounterbit_6_carryout), .CarryOut(downcounterbit_7_carryout));  // open: n_CntOut, CntOut
  DownCounterBit downcounterbit_8 (
    .n_ACLK(n_ACLK), .Load(WriteEn), .Value(LC[7]), .Clear(RES), .Step(STEP),
    .CarryIn(downcounterbit_7_carryout), .CarryOut(CarryOut));  // open: n_CntOut, CntOut
endmodule

module LengthCounters (
  input  ACLK,
  input  n_ACLK,
  input  RES,
  input  W4015,
  input  n_R4015,
  input  W4003,
  input  W4007,
  input  W400B,
  input  W400F,
  input  [7:0] DB_In,
  input  n_LFO2,
  input  SQA_LC,
  input  SQB_LC,
  input  TRI_LC,
  input  RND_LC,
  output [7:0] DB_Out,
  output NOSQA,
  output NOSQB,
  output NOTRI,
  output NORND
);

  wire RND_cnt8_carryout, RND_ctrl_step, SQA_cnt8_carryout, SQA_ctrl_step, SQB_cnt8_carryout, SQB_ctrl_step,
       TRI_cnt8_carryout, TRI_ctrl_step;
  wire [7:0] lc_dec_lc;

  Length_Decoder lc_dec (.DB(DB_In), .LC(lc_dec_lc));
  Length_Counter SQA_cnt8 (
    .n_ACLK(n_ACLK), .STEP(SQA_ctrl_step), .RES(RES), .WriteEn(W4003), .LC(lc_dec_lc), .CarryIn(SQA_LC),
    .CarryOut(SQA_cnt8_carryout));
  Length_Control SQA_ctrl (
    .ACLK(ACLK), .n_ACLK(n_ACLK), .RES(RES), .n_LFO2(n_LFO2), .W4015(W4015), .WriteEn(W4003),
    .n_R4015(n_R4015), .DB_Bit_in(DB_In[0]), .CarryOut(SQA_cnt8_carryout), .NO_LC(NOSQA),
    .DB_Bit_out(DB_Out[0]), .STEP(SQA_ctrl_step));
  Length_Counter SQB_cnt8 (
    .n_ACLK(n_ACLK), .STEP(SQB_ctrl_step), .RES(RES), .WriteEn(W4007), .LC(lc_dec_lc), .CarryIn(SQB_LC),
    .CarryOut(SQB_cnt8_carryout));
  Length_Control SQB_ctrl (
    .ACLK(ACLK), .n_ACLK(n_ACLK), .RES(RES), .n_LFO2(n_LFO2), .W4015(W4015), .WriteEn(W4007),
    .n_R4015(n_R4015), .DB_Bit_in(DB_In[1]), .CarryOut(SQB_cnt8_carryout), .NO_LC(NOSQB),
    .DB_Bit_out(DB_Out[1]), .STEP(SQB_ctrl_step));
  Length_Counter TRI_cnt8 (
    .n_ACLK(n_ACLK), .STEP(TRI_ctrl_step), .RES(RES), .WriteEn(W400B), .LC(lc_dec_lc), .CarryIn(TRI_LC),
    .CarryOut(TRI_cnt8_carryout));
  Length_Control TRI_ctrl (
    .ACLK(ACLK), .n_ACLK(n_ACLK), .RES(RES), .n_LFO2(n_LFO2), .W4015(W4015), .WriteEn(W400B),
    .n_R4015(n_R4015), .DB_Bit_in(DB_In[2]), .CarryOut(TRI_cnt8_carryout), .NO_LC(NOTRI),
    .DB_Bit_out(DB_Out[2]), .STEP(TRI_ctrl_step));
  Length_Counter RND_cnt8 (
    .n_ACLK(n_ACLK), .STEP(RND_ctrl_step), .RES(RES), .WriteEn(W400F), .LC(lc_dec_lc), .CarryIn(RND_LC),
    .CarryOut(RND_cnt8_carryout));
  Length_Control RND_ctrl (
    .ACLK(ACLK), .n_ACLK(n_ACLK), .RES(RES), .n_LFO2(n_LFO2), .W4015(W4015), .WriteEn(W400F),
    .n_R4015(n_R4015), .DB_Bit_in(DB_In[3]), .CarryOut(RND_cnt8_carryout), .NO_LC(NORND),
    .DB_Bit_out(DB_Out[3]), .STEP(RND_ctrl_step));

  // Notes on the sheet:
  //   write enablers
  //   Carries in
endmodule
module SQUARE (
  input  ACLK,
  input  n_ACLK,
  input  RES,
  input  WR0,
  input  WR1,
  input  WR2,
  input  WR3,
  input  n_LFO1,
  input  n_LFO2,
  input  NOSQ,
  input  LOCK,
  input  CarryMode,
  input  [7:0] DB_in,
  output SQ_LC,
  output [3:0] SQ_Out
);

  wire adder_n_cout, adder_sw_uvf, DEC, dir_reg_n_valout, duty_unit_duty, freq_cnt_fco, freq_cnt_fload, INC,
       sweep_unit_do_sweep, sweep_unit_sw_ovf;
  wire [2:0] shift_reg_sr;
  wire [3:0] env_unit_v;
  wire [10:0] adder_n_sum, barrel_s, freq_reg_fx, freq_reg_nfx, multiplexer_1_out;

  SQUARE_FreqReg freq_reg (
    .ACLK(ACLK), .n_ACLK(n_ACLK), .WR2(WR2), .WR3(WR3), .DB_in(DB_in), .DO_SWEEP(sweep_unit_do_sweep),
    .n_sum(adder_n_sum), .nFx(freq_reg_nfx), .Fx(freq_reg_fx));
  SQUARE_ShiftReg shift_reg (.n_ACLK(n_ACLK), .WR1(WR1), .DB_in(DB_in), .SR(shift_reg_sr));
  RegisterBit dir_reg (.n_ACLK(n_ACLK), .Enable(WR1), .Value(DB_in[3]), .ValOut(DEC), .n_ValOut(dir_reg_n_valout));
  // NoConnect on dir_reg_n_valout
  not not_1 (INC, DEC);
  Multiplexer #(.width(11)) multiplexer_1 (.in0(freq_reg_fx), .in1(freq_reg_nfx), .out(multiplexer_1_out), .sel(DEC));
  SQUARE_Sweep sweep_unit (
    .n_ACLK(n_ACLK), .RES(RES), .WR1(WR1), .SR(shift_reg_sr), .DEC(DEC), .n_COUT(adder_n_cout),
    .SW_UVF(adder_sw_uvf), .NOSQ(NOSQ), .n_LFO2(n_LFO2), .DB_in(DB_in), .DO_SWEEP(sweep_unit_do_sweep),
    .SW_OVF(sweep_unit_sw_ovf));
  SQUARE_Adder adder (
    .CarryMode(CarryMode), .INC(INC), .nFx(freq_reg_nfx), .Fx(freq_reg_fx), .S(barrel_s),
    .n_sum(adder_n_sum), .n_COUT(adder_n_cout), .SW_UVF(adder_sw_uvf));
  SQUARE_BarrelShifter barrel (.BS({DEC, multiplexer_1_out}), .SR(shift_reg_sr), .S(barrel_s));
  SQUARE_FreqCounter freq_cnt (
    .ACLK(ACLK), .n_ACLK(n_ACLK), .RES(RES), .Fx(freq_reg_fx), .FCO(freq_cnt_fco), .FLOAD(freq_cnt_fload));
  EnvelopeUnit env_unit (
    .n_ACLK(n_ACLK), .RES(RES), .WR_Reg(WR0), .WR_LC(WR3), .n_LFO1(n_LFO1), .DB_in(DB_in), .V(env_unit_v),
    .LC(SQ_LC));
  SQUARE_Duty duty_unit (
    .n_ACLK(n_ACLK), .RES(RES), .FLOAD(freq_cnt_fload), .FCO(freq_cnt_fco), .WR0(WR0), .WR3(WR3),
    .DB_in(DB_in), .DUTY(duty_unit_duty));
  SQUARE_Output sqo (
    .n_ACLK(n_ACLK), .DUTY(duty_unit_duty), .LOCK(LOCK), .SW_UVF(adder_sw_uvf), .NOSQ(NOSQ),
    .SW_OVF(sweep_unit_sw_ovf), .V(env_unit_v), .SQ_Out(SQ_Out));
endmodule

module TRIANGLE (
  input  PHI1,
  input  n_ACLK,
  input  RES,
  input  W4008,
  input  W400A,
  input  W400B,
  input  W401A,
  input  n_LFO1,
  input  NOTRI,
  input  LOCK,
  input  [7:0] DB_in,
  output TRI_LC,
  output [3:0] TRI_Out
);

  wire ctrl_load, ctrl_step, ctrl_tstep, freq_cnt_n_fout, lin_cnt_tco;

  TRIANGLE_Control ctrl (
    .PHI1(PHI1), .n_ACLK(n_ACLK), .W4008(W4008), .W400B(W400B), .n_LFO1(n_LFO1), .NOTRI(NOTRI), .LOCK(LOCK),
    .TCO(lin_cnt_tco), .n_FOUT(freq_cnt_n_fout), .DB_in(DB_in), .TRI_LC(TRI_LC), .LOAD(ctrl_load),
    .STEP(ctrl_step), .TSTEP(ctrl_tstep));
  TRIANGLE_LinearCounter lin_cnt (
    .n_ACLK(n_ACLK), .RES(RES), .W4008(W4008), .LOAD(ctrl_load), .STEP(ctrl_step), .DB_in(DB_in),
    .TCO(lin_cnt_tco));
  TRIANGLE_FreqCounter freq_cnt (
    .PHI1(PHI1), .RES(RES), .W400A(W400A), .W400B(W400B), .DB_in(DB_in), .n_FOUT(freq_cnt_n_fout));
  TRIANGLE_Output tria_out (
    .PHI1(PHI1), .RES(RES), .W401A(W401A), .TSTEP(ctrl_tstep), .DB_in(DB_in), .TRIA_Out(TRI_Out));
endmodule

module NOISE (
  input  ACLK,
  input  n_ACLK,
  input  RES,
  input  W400C,
  input  W400E,
  input  W400F,
  input  n_LFO1,
  input  NORND,
  input  LOCK,
  input  [7:0] DB_in,
  output RND_LC,
  output [3:0] RND_Out
);

  wire freq_lfsr_rstep, rnd_lfsr_rndout;
  wire [3:0] bit_extender_1_out, env_unit_v, freq_reg_nfx, not_1_out;
  wire [10:0] dec_nnfx;

  NOISE_FreqReg freq_reg (.n_ACLK(n_ACLK), .RES(RES), .W400E(W400E), .DB_in(DB_in), .NFx(freq_reg_nfx));
  NOISE_FreqLFSR freq_lfsr (.ACLK(ACLK), .n_ACLK(n_ACLK), .RES(RES), .NNF(dec_nnfx), .RSTEP(freq_lfsr_rstep));
  NOISE_Decoder dec (.NFx(freq_reg_nfx), .NNFx(dec_nnfx));
  NOISE_RandomLFSR rnd_lfsr (
    .n_ACLK(n_ACLK), .RSTEP(freq_lfsr_rstep), .NORND(NORND), .LOCK(LOCK), .W400E(W400E), .DB_in(DB_in),
    .RNDOUT(rnd_lfsr_rndout));
  EnvelopeUnit env_unit (
    .n_ACLK(n_ACLK), .RES(RES), .WR_Reg(W400C), .WR_LC(W400F), .n_LFO1(n_LFO1), .DB_in(DB_in),
    .V(env_unit_v), .LC(RND_LC));
  assign bit_extender_1_out = {{3{rnd_lfsr_rndout}}, rnd_lfsr_rndout};  // Bit_Extender bit_extender_1
  assign not_1_out = ~env_unit_v;  // NOT_Gate not_1, 4 bits wide
  assign RND_Out = ~(bit_extender_1_out | not_1_out);  // NOR_Gate nor_1, 4 bits wide
endmodule

module DAC_A (
  input  [3:0] SQA,
  input  [3:0] SQB,
  output [31:0] AUX_A
);

  ROM #(.dataWidth(32)) auxa_rom (.addr({SQB, SQA}), .data(AUX_A));
endmodule

module DAC_B (
  input  [3:0] TRIA,
  input  [3:0] RND,
  input  [6:0] DMC,
  output [31:0] AUX_B
);

  ROM #(.addrWidth(15), .dataWidth(32)) auxb_rom (.addr({DMC, RND, TRIA}), .data(AUX_B));
endmodule

module SQUARE_FreqReg (
  input  ACLK,
  input  n_ACLK,
  input  WR2,
  input  WR3,
  input  [7:0] DB_in,
  input  DO_SWEEP,
  input  [10:0] n_sum,
  output [10:0] nFx,
  output [10:0] Fx
);

  SQ_FreqRegBit f0 (
    .ACLK(ACLK), .n_ACLK(n_ACLK), .WR(WR2), .DB_in(DB_in[0]), .DO_SWEEP(DO_SWEEP), .n_sum(n_sum[0]),
    .nFx(nFx[0]), .Fx(Fx[0]));
  SQ_FreqRegBit f1 (
    .ACLK(ACLK), .n_ACLK(n_ACLK), .WR(WR2), .DB_in(DB_in[1]), .DO_SWEEP(DO_SWEEP), .n_sum(n_sum[1]),
    .nFx(nFx[1]), .Fx(Fx[1]));
  SQ_FreqRegBit f2 (
    .ACLK(ACLK), .n_ACLK(n_ACLK), .WR(WR2), .DB_in(DB_in[2]), .DO_SWEEP(DO_SWEEP), .n_sum(n_sum[2]),
    .nFx(nFx[2]), .Fx(Fx[2]));
  SQ_FreqRegBit f3 (
    .ACLK(ACLK), .n_ACLK(n_ACLK), .WR(WR2), .DB_in(DB_in[3]), .DO_SWEEP(DO_SWEEP), .n_sum(n_sum[3]),
    .nFx(nFx[3]), .Fx(Fx[3]));
  SQ_FreqRegBit f4 (
    .ACLK(ACLK), .n_ACLK(n_ACLK), .WR(WR2), .DB_in(DB_in[4]), .DO_SWEEP(DO_SWEEP), .n_sum(n_sum[4]),
    .nFx(nFx[4]), .Fx(Fx[4]));
  SQ_FreqRegBit f5 (
    .ACLK(ACLK), .n_ACLK(n_ACLK), .WR(WR2), .DB_in(DB_in[5]), .DO_SWEEP(DO_SWEEP), .n_sum(n_sum[5]),
    .nFx(nFx[5]), .Fx(Fx[5]));
  SQ_FreqRegBit f6 (
    .ACLK(ACLK), .n_ACLK(n_ACLK), .WR(WR2), .DB_in(DB_in[6]), .DO_SWEEP(DO_SWEEP), .n_sum(n_sum[6]),
    .nFx(nFx[6]), .Fx(Fx[6]));
  SQ_FreqRegBit f7 (
    .ACLK(ACLK), .n_ACLK(n_ACLK), .WR(WR2), .DB_in(DB_in[7]), .DO_SWEEP(DO_SWEEP), .n_sum(n_sum[7]),
    .nFx(nFx[7]), .Fx(Fx[7]));
  SQ_FreqRegBit f8 (
    .ACLK(ACLK), .n_ACLK(n_ACLK), .WR(WR3), .DB_in(DB_in[0]), .DO_SWEEP(DO_SWEEP), .n_sum(n_sum[8]),
    .nFx(nFx[8]), .Fx(Fx[8]));
  SQ_FreqRegBit f9 (
    .ACLK(ACLK), .n_ACLK(n_ACLK), .WR(WR3), .DB_in(DB_in[1]), .DO_SWEEP(DO_SWEEP), .n_sum(n_sum[9]),
    .nFx(nFx[9]), .Fx(Fx[9]));
  SQ_FreqRegBit f10 (
    .ACLK(ACLK), .n_ACLK(n_ACLK), .WR(WR3), .DB_in(DB_in[2]), .DO_SWEEP(DO_SWEEP), .n_sum(n_sum[10]),
    .nFx(nFx[10]), .Fx(Fx[10]));
endmodule

module SQ_FreqRegBit (
  input  ACLK,
  input  n_ACLK,
  input  WR,
  input  DB_in,
  input  DO_SWEEP,
  input  n_sum,
  output nFx,
  output Fx
);

  wire and_1_out, and_2_out, controlled_buffer_1_out, not_1_out, sum_latch_n_valout, sum_latch_valout,
       transp_q;

  not not_1 (not_1_out, ACLK);
  DLatch sum_latch (.Enable(n_ACLK), .Value(n_sum), .ValOut(sum_latch_valout), .n_ValOut(sum_latch_n_valout));
  assign controlled_buffer_1_out = WR ? DB_in : 1'bz;  // Controlled_Buffer controlled_buffer_1
  assign controlled_buffer_1_out = not_1_out ? Fx : 1'bz;  // Controlled_Buffer controlled_buffer_2
  and and_1 (and_1_out, sum_latch_n_valout, DO_SWEEP);
  TranspDLatch transp (.d(controlled_buffer_1_out), .q(transp_q));  // open: nq
  and and_2 (and_2_out, DO_SWEEP, sum_latch_valout);
  nor nor_1 (nFx, and_1_out, transp_q);
  nor nor_2 (Fx, nFx, and_2_out);

  // Notes on the sheet:
  //   /ACLK3
  //   Freq_FF
endmodule

module SQUARE_ShiftReg (
  input  n_ACLK,
  input  WR1,
  input  [7:0] DB_in,
  output [2:0] SR
);

  RegisterBit sr0 (.n_ACLK(n_ACLK), .Enable(WR1), .Value(DB_in[0]), .ValOut(SR[0]));  // open: n_ValOut
  RegisterBit sr1 (.n_ACLK(n_ACLK), .Enable(WR1), .Value(DB_in[1]), .ValOut(SR[1]));  // open: n_ValOut
  RegisterBit sr2 (.n_ACLK(n_ACLK), .Enable(WR1), .Value(DB_in[2]), .ValOut(SR[2]));  // open: n_ValOut
endmodule

module SQUARE_BarrelShifter (
  input  [11:0] BS,
  input  [2:0] SR,
  output [10:0] S
);

  wire multiplexer_1_out, multiplexer_2_out, multiplexer_3_out, multiplexer_4_out, multiplexer_5_out,
       multiplexer_6_out, multiplexer_7_out, multiplexer_8_out, multiplexer_9_out, multiplexer_10_out,
       multiplexer_11_out, multiplexer_12_out, multiplexer_13_out, multiplexer_14_out, multiplexer_15_out,
       multiplexer_16_out, multiplexer_17_out, multiplexer_18_out, multiplexer_19_out, multiplexer_20_out,
       multiplexer_21_out, multiplexer_22_out;

  Multiplexer multiplexer_1 (.in0(BS[0]), .in1(BS[1]), .out(multiplexer_1_out), .sel(SR[0]));
  Multiplexer multiplexer_2 (.in0(BS[1]), .in1(BS[2]), .out(multiplexer_2_out), .sel(SR[0]));
  Multiplexer multiplexer_3 (.in0(BS[2]), .in1(BS[3]), .out(multiplexer_3_out), .sel(SR[0]));
  Multiplexer multiplexer_4 (.in0(BS[3]), .in1(BS[4]), .out(multiplexer_4_out), .sel(SR[0]));
  Multiplexer multiplexer_5 (.in0(BS[4]), .in1(BS[5]), .out(multiplexer_5_out), .sel(SR[0]));
  Multiplexer multiplexer_6 (.in0(BS[5]), .in1(BS[6]), .out(multiplexer_6_out), .sel(SR[0]));
  Multiplexer multiplexer_7 (.in0(BS[6]), .in1(BS[7]), .out(multiplexer_7_out), .sel(SR[0]));
  Multiplexer multiplexer_8 (.in0(BS[7]), .in1(BS[8]), .out(multiplexer_8_out), .sel(SR[0]));
  Multiplexer multiplexer_9 (.in0(BS[8]), .in1(BS[9]), .out(multiplexer_9_out), .sel(SR[0]));
  Multiplexer multiplexer_10 (.in0(BS[9]), .in1(BS[10]), .out(multiplexer_10_out), .sel(SR[0]));
  Multiplexer multiplexer_11 (.in0(BS[10]), .in1(BS[11]), .out(multiplexer_11_out), .sel(SR[0]));
  Multiplexer multiplexer_12 (.in0(multiplexer_1_out), .in1(multiplexer_3_out), .out(multiplexer_12_out), .sel(SR[1]));
  Multiplexer multiplexer_13 (.in0(multiplexer_2_out), .in1(multiplexer_4_out), .out(multiplexer_13_out), .sel(SR[1]));
  Multiplexer multiplexer_14 (.in0(multiplexer_3_out), .in1(multiplexer_5_out), .out(multiplexer_14_out), .sel(SR[1]));
  Multiplexer multiplexer_15 (.in0(multiplexer_4_out), .in1(multiplexer_6_out), .out(multiplexer_15_out), .sel(SR[1]));
  Multiplexer multiplexer_16 (.in0(multiplexer_5_out), .in1(multiplexer_7_out), .out(multiplexer_16_out), .sel(SR[1]));
  Multiplexer multiplexer_17 (.in0(multiplexer_6_out), .in1(multiplexer_8_out), .out(multiplexer_17_out), .sel(SR[1]));
  Multiplexer multiplexer_18 (.in0(multiplexer_7_out), .in1(multiplexer_9_out), .out(multiplexer_18_out), .sel(SR[1]));
  Multiplexer multiplexer_19 (.in0(multiplexer_8_out), .in1(multiplexer_10_out), .out(multiplexer_19_out), .sel(SR[1]));
  Multiplexer multiplexer_20 (.in0(multiplexer_9_out), .in1(multiplexer_11_out), .out(multiplexer_20_out), .sel(SR[1]));
  Multiplexer multiplexer_21 (.in0(multiplexer_10_out), .in1(BS[11]), .out(multiplexer_21_out), .sel(SR[1]));
  Multiplexer multiplexer_22 (.in0(multiplexer_11_out), .in1(BS[11]), .out(multiplexer_22_out), .sel(SR[1]));
  Multiplexer multiplexer_23 (.in0(multiplexer_12_out), .in1(multiplexer_16_out), .out(S[0]), .sel(SR[2]));
  Multiplexer multiplexer_24 (.in0(multiplexer_13_out), .in1(multiplexer_17_out), .out(S[1]), .sel(SR[2]));
  Multiplexer multiplexer_25 (.in0(multiplexer_14_out), .in1(multiplexer_18_out), .out(S[2]), .sel(SR[2]));
  Multiplexer multiplexer_26 (.in0(multiplexer_15_out), .in1(multiplexer_19_out), .out(S[3]), .sel(SR[2]));
  Multiplexer multiplexer_27 (.in0(multiplexer_16_out), .in1(multiplexer_20_out), .out(S[4]), .sel(SR[2]));
  Multiplexer multiplexer_28 (.in0(multiplexer_17_out), .in1(multiplexer_21_out), .out(S[5]), .sel(SR[2]));
  Multiplexer multiplexer_29 (.in0(multiplexer_18_out), .in1(multiplexer_22_out), .out(S[6]), .sel(SR[2]));
  Multiplexer multiplexer_30 (.in0(multiplexer_19_out), .in1(BS[11]), .out(S[7]), .sel(SR[2]));
  Multiplexer multiplexer_31 (.in0(multiplexer_20_out), .in1(BS[11]), .out(S[8]), .sel(SR[2]));
  Multiplexer multiplexer_32 (.in0(multiplexer_21_out), .in1(BS[11]), .out(S[9]), .sel(SR[2]));
  Multiplexer multiplexer_33 (.in0(multiplexer_22_out), .in1(BS[11]), .out(S[10]), .sel(SR[2]));
endmodule

module SQUARE_Adder (
  input  CarryMode,
  input  INC,
  input  [10:0] nFx,
  input  [10:0] Fx,
  input  [10:0] S,
  output [10:0] n_sum,
  output n_COUT,
  output SW_UVF
);

  wire multiplexer_1_out, not_2_out, sq_adderbit_1_cout, sq_adderbit_1_n_cout, sq_adderbit_2_cout,
       sq_adderbit_2_n_cout, sq_adderbit_3_cout, sq_adderbit_3_n_cout, sq_adderbit_4_cout,
       sq_adderbit_4_n_cout, sq_adderbit_5_cout, sq_adderbit_5_n_cout, sq_adderbit_6_cout,
       sq_adderbit_6_n_cout, sq_adderbit_7_cout, sq_adderbit_7_n_cout, sq_adderbit_8_cout,
       sq_adderbit_8_n_cout, sq_adderbit_9_cout, sq_adderbit_9_n_cout, sq_adderbit_10_cout,
       sq_adderbit_10_n_cout, sq_adderbit_11_cout;
  wire [10:0] not_1_out;

  assign not_1_out = ~S;  // NOT_Gate not_1, 11 bits wide
  Multiplexer multiplexer_1 (.in0(INC), .in1(1'b1), .out(multiplexer_1_out), .sel(CarryMode));
  nor nor_1 (SW_UVF, Fx[2], Fx[3], Fx[4], Fx[5], Fx[6], Fx[7], Fx[8], Fx[9], Fx[10]);
  not not_2 (not_2_out, multiplexer_1_out);
  SQ_AdderBit sq_adderbit_1 (
    .F(Fx[0]), .nF(nFx[0]), .S(S[0]), .nS(not_1_out[0]), .C(not_2_out), .nC(multiplexer_1_out),
    .n_cout(sq_adderbit_1_n_cout), .cout(sq_adderbit_1_cout), .n_sum(n_sum[0]));
  SQ_AdderBit sq_adderbit_2 (
    .F(Fx[1]), .nF(nFx[1]), .S(S[1]), .nS(not_1_out[1]), .C(sq_adderbit_1_cout), .nC(sq_adderbit_1_n_cout),
    .n_cout(sq_adderbit_2_n_cout), .cout(sq_adderbit_2_cout), .n_sum(n_sum[1]));
  SQ_AdderBit sq_adderbit_3 (
    .F(Fx[2]), .nF(nFx[2]), .S(S[2]), .nS(not_1_out[2]), .C(sq_adderbit_2_cout), .nC(sq_adderbit_2_n_cout),
    .n_cout(sq_adderbit_3_n_cout), .cout(sq_adderbit_3_cout), .n_sum(n_sum[2]));
  SQ_AdderBit sq_adderbit_4 (
    .F(Fx[3]), .nF(nFx[3]), .S(S[3]), .nS(not_1_out[3]), .C(sq_adderbit_3_cout), .nC(sq_adderbit_3_n_cout),
    .n_cout(sq_adderbit_4_n_cout), .cout(sq_adderbit_4_cout), .n_sum(n_sum[3]));
  SQ_AdderBit sq_adderbit_5 (
    .F(Fx[4]), .nF(nFx[4]), .S(S[4]), .nS(not_1_out[4]), .C(sq_adderbit_4_cout), .nC(sq_adderbit_4_n_cout),
    .n_cout(sq_adderbit_5_n_cout), .cout(sq_adderbit_5_cout), .n_sum(n_sum[4]));
  SQ_AdderBit sq_adderbit_6 (
    .F(Fx[5]), .nF(nFx[5]), .S(S[5]), .nS(not_1_out[5]), .C(sq_adderbit_5_cout), .nC(sq_adderbit_5_n_cout),
    .n_cout(sq_adderbit_6_n_cout), .cout(sq_adderbit_6_cout), .n_sum(n_sum[5]));
  SQ_AdderBit sq_adderbit_7 (
    .F(Fx[6]), .nF(nFx[6]), .S(S[6]), .nS(not_1_out[6]), .C(sq_adderbit_6_cout), .nC(sq_adderbit_6_n_cout),
    .n_cout(sq_adderbit_7_n_cout), .cout(sq_adderbit_7_cout), .n_sum(n_sum[6]));
  SQ_AdderBit sq_adderbit_8 (
    .F(Fx[7]), .nF(nFx[7]), .S(S[7]), .nS(not_1_out[7]), .C(sq_adderbit_7_cout), .nC(sq_adderbit_7_n_cout),
    .n_cout(sq_adderbit_8_n_cout), .cout(sq_adderbit_8_cout), .n_sum(n_sum[7]));
  SQ_AdderBit sq_adderbit_9 (
    .F(Fx[8]), .nF(nFx[8]), .S(S[8]), .nS(not_1_out[8]), .C(sq_adderbit_8_cout), .nC(sq_adderbit_8_n_cout),
    .n_cout(sq_adderbit_9_n_cout), .cout(sq_adderbit_9_cout), .n_sum(n_sum[8]));
  SQ_AdderBit sq_adderbit_10 (
    .F(Fx[9]), .nF(nFx[9]), .S(S[9]), .nS(not_1_out[9]), .C(sq_adderbit_9_cout), .nC(sq_adderbit_9_n_cout),
    .n_cout(sq_adderbit_10_n_cout), .cout(sq_adderbit_10_cout), .n_sum(n_sum[9]));
  SQ_AdderBit sq_adderbit_11 (
    .F(Fx[10]), .nF(nFx[10]), .S(S[10]), .nS(not_1_out[10]), .C(sq_adderbit_10_cout),
    .nC(sq_adderbit_10_n_cout), .n_cout(n_COUT), .cout(sq_adderbit_11_cout), .n_sum(n_sum[10]));
  // NoConnect on sq_adderbit_11_cout
endmodule

module SQ_AdderBit (
  input  F,
  input  nF,
  input  S,
  input  nS,
  input  C,
  input  nC,
  output n_cout,
  output cout,
  output n_sum
);

  wire and_1_out, and_2_out, and_3_out, and_4_out, and_5_out, and_6_out, and_7_out;

  and and_1 (and_1_out, F, S);
  and and_2 (and_2_out, F, C, nS);
  and and_3 (and_3_out, C, nF, S);
  and and_4 (and_4_out, nC, F, nS);
  and and_5 (and_5_out, nC, nF, S);
  and and_6 (and_6_out, C, nF, nS);
  and and_7 (and_7_out, F, C, S);
  nor nor_1 (n_cout, and_1_out, and_2_out, and_3_out);
  nor nor_2 (n_sum, and_4_out, and_5_out, and_6_out, and_7_out);
  not not_1 (cout, n_cout);
endmodule

module SQUARE_FreqCounter (
  input  ACLK,
  input  n_ACLK,
  input  RES,
  input  [10:0] Fx,
  output FCO,
  output FLOAD
);

  wire downcounterbit_1_carryout, downcounterbit_2_carryout, downcounterbit_3_carryout,
       downcounterbit_4_carryout, downcounterbit_5_carryout, downcounterbit_6_carryout,
       downcounterbit_7_carryout, downcounterbit_8_carryout, downcounterbit_9_carryout,
       downcounterbit_10_carryout, fco_latch_n_valout, nor_2_out, not_1_out;

  DLatch fco_latch (.Enable(n_ACLK), .Value(FCO), .n_ValOut(fco_latch_n_valout));  // open: ValOut
  not not_1 (not_1_out, fco_latch_n_valout);
  nor nor_1 (FLOAD, ACLK, fco_latch_n_valout);
  nor nor_2 (nor_2_out, ACLK, not_1_out);
  DownCounterBit downcounterbit_1 (
    .n_ACLK(n_ACLK), .Load(FLOAD), .Value(Fx[0]), .Clear(RES), .Step(nor_2_out), .CarryIn(1'b1),
    .CarryOut(downcounterbit_1_carryout));  // open: n_CntOut, CntOut
  DownCounterBit downcounterbit_2 (
    .n_ACLK(n_ACLK), .Load(FLOAD), .Value(Fx[1]), .Clear(RES), .Step(nor_2_out),
    .CarryIn(downcounterbit_1_carryout), .CarryOut(downcounterbit_2_carryout));  // open: n_CntOut, CntOut
  DownCounterBit downcounterbit_3 (
    .n_ACLK(n_ACLK), .Load(FLOAD), .Value(Fx[2]), .Clear(RES), .Step(nor_2_out),
    .CarryIn(downcounterbit_2_carryout), .CarryOut(downcounterbit_3_carryout));  // open: n_CntOut, CntOut
  DownCounterBit downcounterbit_4 (
    .n_ACLK(n_ACLK), .Load(FLOAD), .Value(Fx[3]), .Clear(RES), .Step(nor_2_out),
    .CarryIn(downcounterbit_3_carryout), .CarryOut(downcounterbit_4_carryout));  // open: n_CntOut, CntOut
  DownCounterBit downcounterbit_5 (
    .n_ACLK(n_ACLK), .Load(FLOAD), .Value(Fx[4]), .Clear(RES), .Step(nor_2_out),
    .CarryIn(downcounterbit_4_carryout), .CarryOut(downcounterbit_5_carryout));  // open: n_CntOut, CntOut
  DownCounterBit downcounterbit_6 (
    .n_ACLK(n_ACLK), .Load(FLOAD), .Value(Fx[5]), .Clear(RES), .Step(nor_2_out),
    .CarryIn(downcounterbit_5_carryout), .CarryOut(downcounterbit_6_carryout));  // open: n_CntOut, CntOut
  DownCounterBit downcounterbit_7 (
    .n_ACLK(n_ACLK), .Load(FLOAD), .Value(Fx[6]), .Clear(RES), .Step(nor_2_out),
    .CarryIn(downcounterbit_6_carryout), .CarryOut(downcounterbit_7_carryout));  // open: n_CntOut, CntOut
  DownCounterBit downcounterbit_8 (
    .n_ACLK(n_ACLK), .Load(FLOAD), .Value(Fx[7]), .Clear(RES), .Step(nor_2_out),
    .CarryIn(downcounterbit_7_carryout), .CarryOut(downcounterbit_8_carryout));  // open: n_CntOut, CntOut
  DownCounterBit downcounterbit_9 (
    .n_ACLK(n_ACLK), .Load(FLOAD), .Value(Fx[8]), .Clear(RES), .Step(nor_2_out),
    .CarryIn(downcounterbit_8_carryout), .CarryOut(downcounterbit_9_carryout));  // open: n_CntOut, CntOut
  DownCounterBit downcounterbit_10 (
    .n_ACLK(n_ACLK), .Load(FLOAD), .Value(Fx[9]), .Clear(RES), .Step(nor_2_out),
    .CarryIn(downcounterbit_9_carryout), .CarryOut(downcounterbit_10_carryout));  // open: n_CntOut, CntOut
  DownCounterBit downcounterbit_11 (
    .n_ACLK(n_ACLK), .Load(FLOAD), .Value(Fx[10]), .Clear(RES), .Step(nor_2_out),
    .CarryIn(downcounterbit_10_carryout), .CarryOut(FCO));  // open: n_CntOut, CntOut

  // Notes on the sheet:
  //   FLOAD
  //   FSTEP
endmodule

module EnvelopeUnit (
  input  n_ACLK,
  input  RES,
  input  WR_Reg,
  input  WR_LC,
  input  n_LFO1,
  input  [7:0] DB_in,
  output [3:0] V,
  output LC
);

  wire and_1_out, downcounterbit_1_carryout, downcounterbit_2_carryout, downcounterbit_3_carryout,
       downcounterbit_4_carryout, downcounterbit_5_carryout, downcounterbit_6_carryout,
       downcounterbit_7_carryout, downcounterbit_8_carryout, eco_latch_valout, envdis_reg_valout,
       erld_latch_valout, nand_1_out, nor_1_out, nor_2_out, nor_3_out, nor_4_out, nor_5_out, nor_6_out,
       nor_7_out, nor_8_out, nor_9_out, not_1_out, not_2_out, rco_latch_n_valout, rco_latch_valout,
       reload_latch_valout;
  wire [3:0] downcounterbit_5_cntout, vol_reg0_valout;

  nor nor_1 (nor_1_out, n_LFO1, erld_latch_valout);
  nor nor_2 (nor_2_out, nor_1_out, nor_3_out);
  DLatch erld_latch (.Enable(n_ACLK), .Value(nor_3_out), .ValOut(erld_latch_valout));  // open: n_ValOut
  nor nor_3 (nor_3_out, nor_2_out, WR_LC);
  RegisterBit vol_reg0 (
    .n_ACLK(n_ACLK), .Enable(WR_Reg), .Value(DB_in[0]), .ValOut(vol_reg0_valout[0]));  // open: n_ValOut
  RegisterBit vol_reg1 (
    .n_ACLK(n_ACLK), .Enable(WR_Reg), .Value(DB_in[1]), .ValOut(vol_reg0_valout[1]));  // open: n_ValOut
  RegisterBit vol_reg2 (
    .n_ACLK(n_ACLK), .Enable(WR_Reg), .Value(DB_in[2]), .ValOut(vol_reg0_valout[2]));  // open: n_ValOut
  RegisterBit vol_reg3 (
    .n_ACLK(n_ACLK), .Enable(WR_Reg), .Value(DB_in[3]), .ValOut(vol_reg0_valout[3]));  // open: n_ValOut
  RegisterBit envdis_reg (
    .n_ACLK(n_ACLK), .Enable(WR_Reg), .Value(DB_in[4]), .ValOut(envdis_reg_valout));  // open: n_ValOut
  RegisterBit lc_reg (.n_ACLK(n_ACLK), .Enable(WR_Reg), .Value(DB_in[5]), .n_ValOut(LC));  // open: ValOut
  DLatch rco_latch (.Enable(n_ACLK), .Value(nor_4_out), .ValOut(rco_latch_valout), .n_ValOut(rco_latch_n_valout));
  nor nor_4 (nor_4_out, downcounterbit_4_carryout, nor_2_out);
  DownCounterBit downcounterbit_1 (
    .n_ACLK(n_ACLK), .Load(nor_5_out), .Value(vol_reg0_valout[0]), .Clear(RES), .Step(nor_6_out),
    .CarryIn(1'b1), .CarryOut(downcounterbit_1_carryout));  // open: n_CntOut, CntOut
  DownCounterBit downcounterbit_2 (
    .n_ACLK(n_ACLK), .Load(nor_5_out), .Value(vol_reg0_valout[1]), .Clear(RES), .Step(nor_6_out),
    .CarryIn(downcounterbit_1_carryout), .CarryOut(downcounterbit_2_carryout));  // open: n_CntOut, CntOut
  DownCounterBit downcounterbit_3 (
    .n_ACLK(n_ACLK), .Load(nor_5_out), .Value(vol_reg0_valout[2]), .Clear(RES), .Step(nor_6_out),
    .CarryIn(downcounterbit_2_carryout), .CarryOut(downcounterbit_3_carryout));  // open: n_CntOut, CntOut
  DownCounterBit downcounterbit_4 (
    .n_ACLK(n_ACLK), .Load(nor_5_out), .Value(vol_reg0_valout[3]), .Clear(RES), .Step(nor_6_out),
    .CarryIn(downcounterbit_3_carryout), .CarryOut(downcounterbit_4_carryout));  // open: n_CntOut, CntOut
  nor nor_5 (nor_5_out, n_LFO1, rco_latch_valout);
  nor nor_6 (nor_6_out, rco_latch_n_valout, n_LFO1);
  DLatch eco_latch (.Enable(n_ACLK), .Value(and_1_out), .ValOut(eco_latch_valout));  // open: n_ValOut
  and and_1 (and_1_out, downcounterbit_8_carryout, ~nor_2_out);  // AND_Gate
  DLatch reload_latch (.Enable(n_ACLK), .Value(nor_2_out), .ValOut(reload_latch_valout));  // open: n_ValOut
  DownCounterBit downcounterbit_5 (
    .n_ACLK(n_ACLK), .Load(nor_9_out), .Value(nand_1_out), .Clear(RES), .Step(nor_8_out), .CarryIn(1'b1),
    .CarryOut(downcounterbit_5_carryout), .CntOut(downcounterbit_5_cntout[0]));  // open: n_CntOut
  DownCounterBit downcounterbit_6 (
    .n_ACLK(n_ACLK), .Load(nor_9_out), .Value(nand_1_out), .Clear(RES), .Step(nor_8_out),
    .CarryIn(downcounterbit_5_carryout), .CarryOut(downcounterbit_6_carryout),
    .CntOut(downcounterbit_5_cntout[1]));  // open: n_CntOut
  DownCounterBit downcounterbit_7 (
    .n_ACLK(n_ACLK), .Load(nor_9_out), .Value(nand_1_out), .Clear(RES), .Step(nor_8_out),
    .CarryIn(downcounterbit_6_carryout), .CarryOut(downcounterbit_7_carryout),
    .CntOut(downcounterbit_5_cntout[2]));  // open: n_CntOut
  DownCounterBit downcounterbit_8 (
    .n_ACLK(n_ACLK), .Load(nor_9_out), .Value(nand_1_out), .Clear(RES), .Step(nor_8_out),
    .CarryIn(downcounterbit_7_carryout), .CarryOut(downcounterbit_8_carryout),
    .CntOut(downcounterbit_5_cntout[3]));  // open: n_CntOut
  nand nand_1 (nand_1_out, eco_latch_valout, LC);
  nor nor_7 (nor_7_out, eco_latch_valout, reload_latch_valout);
  not not_1 (not_1_out, nor_5_out);
  not not_2 (not_2_out, nor_7_out);
  nor nor_8 (nor_8_out, not_1_out, not_2_out);
  nor nor_9 (nor_9_out, not_1_out, nor_7_out);
  Multiplexer #(.width(4)) multiplexer_1 (
    .in0(downcounterbit_5_cntout), .in1(vol_reg0_valout), .out(V), .sel(envdis_reg_valout));

  // Notes on the sheet:
  //   EnvReload_FF
  //   RELOAD
  //   ENVDIS
  //   XXX_LC
  //   VOL
  //   Decay Control
  //   RCO
  //   RLOAD
  //   RSTEP
  //   Envelope Control
  //   RLOAD
  //   ECO
  //   EIN
  //   ENV
  //   ESTEP
  //   ERES
endmodule

module SQUARE_Sweep (
  input  n_ACLK,
  input  RES,
  input  WR1,
  input  [2:0] SR,
  input  DEC,
  input  n_COUT,
  input  SW_UVF,
  input  NOSQ,
  input  n_LFO2,
  input  [7:0] DB_in,
  output DO_SWEEP,
  output SW_OVF
);

  wire downcounterbit_1_carryout, downcounterbit_1_cntout, downcounterbit_1_n_cntout,
       downcounterbit_2_carryout, downcounterbit_2_cntout, downcounterbit_2_n_cntout,
       downcounterbit_3_cntout, downcounterbit_3_n_cntout, nor_1_out, nor_3_out, nor_4_out, nor_5_out,
       nor_6_out, nor_7_out, nor_8_out, not_1_out, reload_latch_n_valout, reload_latch_valout, SCO,
       sco_latch_n_valout, sco_latch_valout, swdis_reg_n_valout, swdis_reg_valout, sweep_reg0_n_valout,
       sweep_reg0_valout, sweep_reg1_n_valout, sweep_reg1_valout, sweep_reg2_n_valout, sweep_reg2_valout;

  nor nor_1 (nor_1_out, SR[0], SR[1], SR[2]);
  nor nor_2 (SW_OVF, DEC, n_COUT);
  DLatch reload_latch (
    .Enable(n_ACLK), .Value(nor_5_out), .ValOut(reload_latch_valout), .n_ValOut(reload_latch_n_valout));
  nor nor_3 (nor_3_out, n_LFO2, reload_latch_valout);
  RegisterBit swdis_reg (
    .n_ACLK(n_ACLK), .Enable(WR1), .Value(DB_in[7]), .ValOut(swdis_reg_valout), .n_ValOut(swdis_reg_n_valout));
  nor nor_4 (nor_4_out, nor_3_out, nor_5_out);
  nor nor_5 (nor_5_out, nor_4_out, WR1);
  RegisterBit sweep_reg0 (
    .n_ACLK(n_ACLK), .Enable(WR1), .Value(DB_in[4]), .ValOut(sweep_reg0_valout),
    .n_ValOut(sweep_reg0_n_valout));
  // NoConnect on sweep_reg0_n_valout
  RegisterBit sweep_reg1 (
    .n_ACLK(n_ACLK), .Enable(WR1), .Value(DB_in[5]), .ValOut(sweep_reg1_valout),
    .n_ValOut(sweep_reg1_n_valout));
  // NoConnect on sweep_reg1_n_valout
  RegisterBit sweep_reg2 (
    .n_ACLK(n_ACLK), .Enable(WR1), .Value(DB_in[6]), .ValOut(sweep_reg2_valout),
    .n_ValOut(sweep_reg2_n_valout));
  // NoConnect on sweep_reg2_n_valout
  // NoConnect on swdis_reg_valout
  DLatch sco_latch (.Enable(n_ACLK), .Value(SCO), .ValOut(sco_latch_valout), .n_ValOut(sco_latch_n_valout));
  nor nor_6 (nor_6_out, reload_latch_n_valout, sco_latch_valout);
  not not_1 (not_1_out, nor_6_out);
  nor nor_7 (nor_7_out, n_LFO2, not_1_out);
  nor nor_8 (nor_8_out, n_LFO2, nor_6_out);
  DownCounterBit downcounterbit_1 (
    .n_ACLK(n_ACLK), .Load(nor_8_out), .Value(sweep_reg0_valout), .Clear(RES), .Step(nor_7_out),
    .CarryIn(1'b1), .CarryOut(downcounterbit_1_carryout), .n_CntOut(downcounterbit_1_n_cntout),
    .CntOut(downcounterbit_1_cntout));
  // NoConnect on downcounterbit_1_n_cntout
  // NoConnect on downcounterbit_1_cntout
  DownCounterBit downcounterbit_2 (
    .n_ACLK(n_ACLK), .Load(nor_8_out), .Value(sweep_reg1_valout), .Clear(RES), .Step(nor_7_out),
    .CarryIn(downcounterbit_1_carryout), .CarryOut(downcounterbit_2_carryout),
    .n_CntOut(downcounterbit_2_n_cntout), .CntOut(downcounterbit_2_cntout));
  // NoConnect on downcounterbit_2_n_cntout
  // NoConnect on downcounterbit_2_cntout
  DownCounterBit downcounterbit_3 (
    .n_ACLK(n_ACLK), .Load(nor_8_out), .Value(sweep_reg2_valout), .Clear(RES), .Step(nor_7_out),
    .CarryIn(downcounterbit_2_carryout), .CarryOut(SCO), .n_CntOut(downcounterbit_3_n_cntout),
    .CntOut(downcounterbit_3_cntout));
  // NoConnect on downcounterbit_3_n_cntout
  // NoConnect on downcounterbit_3_cntout
  nor nor_9 (DO_SWEEP, nor_1_out, swdis_reg_n_valout, NOSQ, SW_OVF, sco_latch_n_valout, n_LFO2, SW_UVF);

  // Notes on the sheet:
  //   SRZ
  //   Reload_FF
  //   SWDIS
  //   SWRELOAD
  //   SSTEP
  //   SLOAD
  //   /SCO
endmodule

module SQUARE_Duty (
  input  n_ACLK,
  input  RES,
  input  FLOAD,
  input  FCO,
  input  WR0,
  input  WR3,
  input  [7:0] DB_in,
  output DUTY
);

  wire downcounterbit_1_carryout, downcounterbit_1_cntout, downcounterbit_1_n_cntout,
       downcounterbit_2_carryout, downcounterbit_2_cntout, downcounterbit_2_n_cntout,
       downcounterbit_3_carryout, downcounterbit_3_cntout, downcounterbit_3_n_cntout, duty_reg0_n_valout,
       duty_reg1_n_valout, nand_1_out, nor_1_out, not_1_out, not_2_out;
  wire [1:0] duty_reg0_valout;

  DownCounterBit downcounterbit_1 (
    .n_ACLK(n_ACLK), .Load(WR3), .Value(1'b0), .Clear(RES), .Step(FLOAD), .CarryIn(FCO),
    .CarryOut(downcounterbit_1_carryout), .n_CntOut(downcounterbit_1_n_cntout),
    .CntOut(downcounterbit_1_cntout));
  // NoConnect on downcounterbit_1_n_cntout
  DownCounterBit downcounterbit_2 (
    .n_ACLK(n_ACLK), .Load(WR3), .Value(1'b0), .Clear(RES), .Step(FLOAD),
    .CarryIn(downcounterbit_1_carryout), .CarryOut(downcounterbit_2_carryout),
    .n_CntOut(downcounterbit_2_n_cntout), .CntOut(downcounterbit_2_cntout));
  // NoConnect on downcounterbit_2_n_cntout
  // NoConnect on downcounterbit_3_carryout
  DownCounterBit downcounterbit_3 (
    .n_ACLK(n_ACLK), .Load(WR3), .Value(1'b0), .Clear(RES), .Step(FLOAD),
    .CarryIn(downcounterbit_2_carryout), .CarryOut(downcounterbit_3_carryout),
    .n_CntOut(downcounterbit_3_n_cntout), .CntOut(downcounterbit_3_cntout));
  // NoConnect on downcounterbit_3_n_cntout
  RegisterBit duty_reg0 (
    .n_ACLK(n_ACLK), .Enable(WR0), .Value(DB_in[6]), .ValOut(duty_reg0_valout[0]),
    .n_ValOut(duty_reg0_n_valout));
  // NoConnect on duty_reg0_n_valout
  RegisterBit duty_reg1 (
    .n_ACLK(n_ACLK), .Enable(WR0), .Value(DB_in[7]), .ValOut(duty_reg0_valout[1]),
    .n_ValOut(duty_reg1_n_valout));
  // NoConnect on duty_reg1_n_valout
  not not_1 (not_1_out, downcounterbit_1_cntout);
  nor nor_1 (nor_1_out, not_1_out, nand_1_out);
  not not_2 (not_2_out, nand_1_out);
  nand nand_1 (nand_1_out, downcounterbit_2_cntout, downcounterbit_3_cntout);
  Multiplexer #(.select(2)) multiplexer_1 (
    .in0(nor_1_out), .in1(not_2_out), .in2(downcounterbit_3_cntout), .in3(nand_1_out), .out(DUTY),
    .sel(duty_reg0_valout));

  // Notes on the sheet:
  //   12.5%
  //   75%
  //   50%
  //   25%
endmodule

module SQUARE_Output (
  input  n_ACLK,
  input  DUTY,
  input  LOCK,
  input  SW_UVF,
  input  NOSQ,
  input  SW_OVF,
  input  [3:0] V,
  output [3:0] SQ_Out
);

  wire nor_1_out, nor_2_out, not_2_out, sqo_latch_valout;
  wire [3:0] bit_extender_1_out, not_1_out;

  assign not_1_out = ~V;  // NOT_Gate not_1, 4 bits wide
  not not_2 (not_2_out, DUTY);
  DLatch sqo_latch (.Enable(n_ACLK), .Value(nor_1_out), .ValOut(sqo_latch_valout));  // open: n_ValOut
  nor nor_1 (nor_1_out, not_2_out, SW_UVF, NOSQ, SW_OVF);
  nor nor_2 (nor_2_out, sqo_latch_valout, LOCK);
  assign bit_extender_1_out = {{3{nor_2_out}}, nor_2_out};  // Bit_Extender bit_extender_1
  assign SQ_Out = ~(bit_extender_1_out | not_1_out);  // NOR_Gate nor_3, 4 bits wide
endmodule

module TRIANGLE_LinearCounter (
  input  n_ACLK,
  input  RES,
  input  W4008,
  input  LOAD,
  input  STEP,
  input  [7:0] DB_in,
  output TCO
);

  wire downcounterbit_1_carryout, downcounterbit_2_carryout, downcounterbit_3_carryout,
       downcounterbit_4_carryout, downcounterbit_5_carryout, downcounterbit_6_carryout, registerbit_1_valout,
       registerbit_2_valout, registerbit_3_valout, registerbit_4_valout, registerbit_5_valout,
       registerbit_6_valout, registerbit_7_valout;

  RegisterBit registerbit_1 (
    .n_ACLK(n_ACLK), .Enable(W4008), .Value(DB_in[0]), .ValOut(registerbit_1_valout));  // open: n_ValOut
  RegisterBit registerbit_2 (
    .n_ACLK(n_ACLK), .Enable(W4008), .Value(DB_in[1]), .ValOut(registerbit_2_valout));  // open: n_ValOut
  RegisterBit registerbit_3 (
    .n_ACLK(n_ACLK), .Enable(W4008), .Value(DB_in[2]), .ValOut(registerbit_3_valout));  // open: n_ValOut
  RegisterBit registerbit_4 (
    .n_ACLK(n_ACLK), .Enable(W4008), .Value(DB_in[3]), .ValOut(registerbit_4_valout));  // open: n_ValOut
  RegisterBit registerbit_5 (
    .n_ACLK(n_ACLK), .Enable(W4008), .Value(DB_in[4]), .ValOut(registerbit_5_valout));  // open: n_ValOut
  RegisterBit registerbit_6 (
    .n_ACLK(n_ACLK), .Enable(W4008), .Value(DB_in[5]), .ValOut(registerbit_6_valout));  // open: n_ValOut
  RegisterBit registerbit_7 (
    .n_ACLK(n_ACLK), .Enable(W4008), .Value(DB_in[6]), .ValOut(registerbit_7_valout));  // open: n_ValOut
  DownCounterBit downcounterbit_1 (
    .n_ACLK(n_ACLK), .Load(LOAD), .Value(registerbit_1_valout), .Clear(RES), .Step(STEP), .CarryIn(1'b1),
    .CarryOut(downcounterbit_1_carryout));  // open: n_CntOut, CntOut
  DownCounterBit downcounterbit_2 (
    .n_ACLK(n_ACLK), .Load(LOAD), .Value(registerbit_2_valout), .Clear(RES), .Step(STEP),
    .CarryIn(downcounterbit_1_carryout), .CarryOut(downcounterbit_2_carryout));  // open: n_CntOut, CntOut
  DownCounterBit downcounterbit_3 (
    .n_ACLK(n_ACLK), .Load(LOAD), .Value(registerbit_3_valout), .Clear(RES), .Step(STEP),
    .CarryIn(downcounterbit_2_carryout), .CarryOut(downcounterbit_3_carryout));  // open: n_CntOut, CntOut
  DownCounterBit downcounterbit_4 (
    .n_ACLK(n_ACLK), .Load(LOAD), .Value(registerbit_4_valout), .Clear(RES), .Step(STEP),
    .CarryIn(downcounterbit_3_carryout), .CarryOut(downcounterbit_4_carryout));  // open: n_CntOut, CntOut
  DownCounterBit downcounterbit_5 (
    .n_ACLK(n_ACLK), .Load(LOAD), .Value(registerbit_5_valout), .Clear(RES), .Step(STEP),
    .CarryIn(downcounterbit_4_carryout), .CarryOut(downcounterbit_5_carryout));  // open: n_CntOut, CntOut
  DownCounterBit downcounterbit_6 (
    .n_ACLK(n_ACLK), .Load(LOAD), .Value(registerbit_6_valout), .Clear(RES), .Step(STEP),
    .CarryIn(downcounterbit_5_carryout), .CarryOut(downcounterbit_6_carryout));  // open: n_CntOut, CntOut
  DownCounterBit downcounterbit_7 (
    .n_ACLK(n_ACLK), .Load(LOAD), .Value(registerbit_7_valout), .Clear(RES), .Step(STEP),
    .CarryIn(downcounterbit_6_carryout), .CarryOut(TCO));  // open: n_CntOut, CntOut
endmodule

module TRIANGLE_FreqCounter (
  input  PHI1,
  input  RES,
  input  W400A,
  input  W400B,
  input  [7:0] DB_in,
  output n_FOUT
);

  wire downcounterbit_1_carryout, downcounterbit_2_carryout, downcounterbit_3_carryout,
       downcounterbit_4_carryout, downcounterbit_5_carryout, downcounterbit_6_carryout,
       downcounterbit_7_carryout, downcounterbit_8_carryout, downcounterbit_9_carryout,
       downcounterbit_10_carryout, downcounterbit_11_carryout, nor_1_out, nor_2_out, not_1_out,
       registerbit_1_valout, registerbit_2_valout, registerbit_3_valout, registerbit_4_valout,
       registerbit_5_valout, registerbit_6_valout, registerbit_7_valout, registerbit_8_valout,
       registerbit_9_valout, registerbit_10_valout, registerbit_11_valout;

  RegisterBit registerbit_1 (
    .n_ACLK(PHI1), .Enable(W400A), .Value(DB_in[0]), .ValOut(registerbit_1_valout));  // open: n_ValOut
  RegisterBit registerbit_2 (
    .n_ACLK(PHI1), .Enable(W400A), .Value(DB_in[1]), .ValOut(registerbit_2_valout));  // open: n_ValOut
  RegisterBit registerbit_3 (
    .n_ACLK(PHI1), .Enable(W400A), .Value(DB_in[2]), .ValOut(registerbit_3_valout));  // open: n_ValOut
  RegisterBit registerbit_4 (
    .n_ACLK(PHI1), .Enable(W400A), .Value(DB_in[3]), .ValOut(registerbit_4_valout));  // open: n_ValOut
  RegisterBit registerbit_5 (
    .n_ACLK(PHI1), .Enable(W400A), .Value(DB_in[4]), .ValOut(registerbit_5_valout));  // open: n_ValOut
  RegisterBit registerbit_6 (
    .n_ACLK(PHI1), .Enable(W400A), .Value(DB_in[5]), .ValOut(registerbit_6_valout));  // open: n_ValOut
  RegisterBit registerbit_7 (
    .n_ACLK(PHI1), .Enable(W400A), .Value(DB_in[6]), .ValOut(registerbit_7_valout));  // open: n_ValOut
  RegisterBit registerbit_8 (
    .n_ACLK(PHI1), .Enable(W400A), .Value(DB_in[7]), .ValOut(registerbit_8_valout));  // open: n_ValOut
  DownCounterBit downcounterbit_1 (
    .n_ACLK(PHI1), .Load(nor_1_out), .Value(registerbit_1_valout), .Clear(RES), .Step(nor_2_out),
    .CarryIn(1'b1), .CarryOut(downcounterbit_1_carryout));  // open: n_CntOut, CntOut
  DownCounterBit downcounterbit_2 (
    .n_ACLK(PHI1), .Load(nor_1_out), .Value(registerbit_2_valout), .Clear(RES), .Step(nor_2_out),
    .CarryIn(downcounterbit_1_carryout), .CarryOut(downcounterbit_2_carryout));  // open: n_CntOut, CntOut
  DownCounterBit downcounterbit_3 (
    .n_ACLK(PHI1), .Load(nor_1_out), .Value(registerbit_3_valout), .Clear(RES), .Step(nor_2_out),
    .CarryIn(downcounterbit_2_carryout), .CarryOut(downcounterbit_3_carryout));  // open: n_CntOut, CntOut
  DownCounterBit downcounterbit_4 (
    .n_ACLK(PHI1), .Load(nor_1_out), .Value(registerbit_4_valout), .Clear(RES), .Step(nor_2_out),
    .CarryIn(downcounterbit_3_carryout), .CarryOut(downcounterbit_4_carryout));  // open: n_CntOut, CntOut
  DownCounterBit downcounterbit_5 (
    .n_ACLK(PHI1), .Load(nor_1_out), .Value(registerbit_5_valout), .Clear(RES), .Step(nor_2_out),
    .CarryIn(downcounterbit_4_carryout), .CarryOut(downcounterbit_5_carryout));  // open: n_CntOut, CntOut
  DownCounterBit downcounterbit_6 (
    .n_ACLK(PHI1), .Load(nor_1_out), .Value(registerbit_6_valout), .Clear(RES), .Step(nor_2_out),
    .CarryIn(downcounterbit_5_carryout), .CarryOut(downcounterbit_6_carryout));  // open: n_CntOut, CntOut
  DownCounterBit downcounterbit_7 (
    .n_ACLK(PHI1), .Load(nor_1_out), .Value(registerbit_7_valout), .Clear(RES), .Step(nor_2_out),
    .CarryIn(downcounterbit_6_carryout), .CarryOut(downcounterbit_7_carryout));  // open: n_CntOut, CntOut
  DownCounterBit downcounterbit_8 (
    .n_ACLK(PHI1), .Load(nor_1_out), .Value(registerbit_8_valout), .Clear(RES), .Step(nor_2_out),
    .CarryIn(downcounterbit_7_carryout), .CarryOut(downcounterbit_8_carryout));  // open: n_CntOut, CntOut
  DLatch dlatch_1 (.Enable(PHI1), .Value(downcounterbit_11_carryout), .n_ValOut(n_FOUT));  // open: ValOut
  not not_1 (not_1_out, n_FOUT);
  RegisterBit registerbit_9 (
    .n_ACLK(PHI1), .Enable(W400B), .Value(DB_in[0]), .ValOut(registerbit_9_valout));  // open: n_ValOut
  RegisterBit registerbit_10 (
    .n_ACLK(PHI1), .Enable(W400B), .Value(DB_in[1]), .ValOut(registerbit_10_valout));  // open: n_ValOut
  RegisterBit registerbit_11 (
    .n_ACLK(PHI1), .Enable(W400B), .Value(DB_in[2]), .ValOut(registerbit_11_valout));  // open: n_ValOut
  nor nor_1 (nor_1_out, PHI1, n_FOUT);
  nor nor_2 (nor_2_out, PHI1, not_1_out);
  DownCounterBit downcounterbit_9 (
    .n_ACLK(PHI1), .Load(nor_1_out), .Value(registerbit_9_valout), .Clear(RES), .Step(nor_2_out),
    .CarryIn(downcounterbit_8_carryout), .CarryOut(downcounterbit_9_carryout));  // open: n_CntOut, CntOut
  DownCounterBit downcounterbit_10 (
    .n_ACLK(PHI1), .Load(nor_1_out), .Value(registerbit_10_valout), .Clear(RES), .Step(nor_2_out),
    .CarryIn(downcounterbit_9_carryout), .CarryOut(downcounterbit_10_carryout));  // open: n_CntOut, CntOut
  DownCounterBit downcounterbit_11 (
    .n_ACLK(PHI1), .Load(nor_1_out), .Value(registerbit_11_valout), .Clear(RES), .Step(nor_2_out),
    .CarryIn(downcounterbit_10_carryout), .CarryOut(downcounterbit_11_carryout));  // open: n_CntOut, CntOut

  // Notes on the sheet:
  //   W400B
  //   FLOAD
  //   FSTEP
endmodule

module TRIANGLE_Control (
  input  PHI1,
  input  n_ACLK,
  input  W4008,
  input  W400B,
  input  n_LFO1,
  input  NOTRI,
  input  LOCK,
  input  TCO,
  input  n_FOUT,
  input  [7:0] DB_in,
  output TRI_LC,
  output LOAD,
  output STEP,
  output TSTEP
);

  wire lc_reg_valout, nor_4_out, nor_5_out, nor_6_out, reload_latch1_valout, reload_latch2_n_valout,
       reload_latch2_valout, tco_latch_valout;

  DLatch reload_latch2 (
    .Enable(n_ACLK), .Value(nor_5_out), .ValOut(reload_latch2_valout), .n_ValOut(reload_latch2_n_valout));
  DLatch tco_latch (.Enable(n_ACLK), .Value(TCO), .ValOut(tco_latch_valout));  // open: n_ValOut
  nor nor_1 (TSTEP, TCO, LOCK, PHI1, NOTRI, n_FOUT);
  RegisterBit lc_reg (.n_ACLK(n_ACLK), .Enable(W4008), .Value(DB_in[7]), .ValOut(lc_reg_valout), .n_ValOut(TRI_LC));
  nor nor_2 (STEP, n_LFO1, reload_latch2_valout, tco_latch_valout);
  nor nor_3 (LOAD, n_LFO1, reload_latch2_n_valout);
  nor nor_4 (nor_4_out, reload_latch1_valout, lc_reg_valout, n_LFO1);
  nor nor_5 (nor_5_out, nor_4_out, nor_6_out);
  DLatch reload_latch1 (.Enable(n_ACLK), .Value(nor_6_out), .ValOut(reload_latch1_valout));  // open: n_ValOut
  nor nor_6 (nor_6_out, nor_5_out, W400B);

  // Notes on the sheet:
  //   Reload_FF
  //   TRELOAD
endmodule

module TRIANGLE_Output (
  input  PHI1,
  input  RES,
  input  W401A,
  input  TSTEP,
  input  [7:0] DB_in,
  output [3:0] TRIA_Out
);

  wire counterbit_1_carryout, counterbit_2_carryout, counterbit_3_carryout, counterbit_4_carryout,
       counterbit_5_carryout, counterbit_5_cntout;
  wire [3:0] counterbit_1_cntout, counterbit_1_n_cntout, multiplexer_1_out;

  CounterBit counterbit_1 (
    .n_ACLK(PHI1), .Load(W401A), .Value(DB_in[0]), .Clear(RES), .Step(TSTEP), .CarryIn(1'b1),
    .CarryOut(counterbit_1_carryout), .n_CntOut(counterbit_1_n_cntout[0]), .CntOut(counterbit_1_cntout[0]));
  CounterBit counterbit_2 (
    .n_ACLK(PHI1), .Load(W401A), .Value(DB_in[1]), .Clear(RES), .Step(TSTEP),
    .CarryIn(counterbit_1_carryout), .CarryOut(counterbit_2_carryout), .n_CntOut(counterbit_1_n_cntout[1]),
    .CntOut(counterbit_1_cntout[1]));
  CounterBit counterbit_3 (
    .n_ACLK(PHI1), .Load(W401A), .Value(DB_in[2]), .Clear(RES), .Step(TSTEP),
    .CarryIn(counterbit_2_carryout), .CarryOut(counterbit_3_carryout), .n_CntOut(counterbit_1_n_cntout[2]),
    .CntOut(counterbit_1_cntout[2]));
  CounterBit counterbit_4 (
    .n_ACLK(PHI1), .Load(W401A), .Value(DB_in[3]), .Clear(RES), .Step(TSTEP),
    .CarryIn(counterbit_3_carryout), .CarryOut(counterbit_4_carryout), .n_CntOut(counterbit_1_n_cntout[3]),
    .CntOut(counterbit_1_cntout[3]));
  // NoConnect on counterbit_5_carryout
  CounterBit counterbit_5 (
    .n_ACLK(PHI1), .Load(W401A), .Value(DB_in[4]), .Clear(RES), .Step(TSTEP),
    .CarryIn(counterbit_4_carryout), .CarryOut(counterbit_5_carryout), .CntOut(counterbit_5_cntout));  // open: n_CntOut
  assign TRIA_Out = ~multiplexer_1_out;  // NOT_Gate not_1, 4 bits wide
  Multiplexer #(.width(4)) multiplexer_1 (
    .in0(counterbit_1_cntout), .in1(counterbit_1_n_cntout), .out(multiplexer_1_out), .sel(counterbit_5_cntout));

  // Notes on the sheet:
  //   T4
  //   q
  //   nq
endmodule

module NOISE_FreqReg (
  input  n_ACLK,
  input  RES,
  input  W400E,
  input  [7:0] DB_in,
  output [3:0] NFx
);

  RegisterBitRes registerbitres_1 (
    .Res(RES), .n_ACLK(n_ACLK), .Enable(W400E), .Value(DB_in[0]), .ValOut(NFx[0]));  // open: n_ValOut
  RegisterBitRes registerbitres_2 (
    .Res(RES), .n_ACLK(n_ACLK), .Enable(W400E), .Value(DB_in[1]), .ValOut(NFx[1]));  // open: n_ValOut
  RegisterBitRes registerbitres_3 (
    .Res(RES), .n_ACLK(n_ACLK), .Enable(W400E), .Value(DB_in[2]), .ValOut(NFx[2]));  // open: n_ValOut
  RegisterBitRes registerbitres_4 (
    .Res(RES), .n_ACLK(n_ACLK), .Enable(W400E), .Value(DB_in[3]), .ValOut(NFx[3]));  // open: n_ValOut
endmodule

module NOISE_Decoder (
  input  [3:0] NFx,
  output [10:0] NNFx
);

  wire [15:0] noise_decoder1_1_dec1_out;

  NOISE_Decoder1 noise_decoder1_1 (.Dec1_in(NFx), .Dec1_out(noise_decoder1_1_dec1_out));
  NOISE_Decoder2 noise_decoder2_1 (.Dec2_in(noise_decoder1_1_dec1_out), .Dec2_out(NNFx));
endmodule

module NOISE_Decoder1 (
  input  [3:0] Dec1_in,
  output [15:0] Dec1_out
);

  wire [3:0] not_1_out;

  assign not_1_out = ~Dec1_in;  // NOT_Gate not_1, 4 bits wide
  nor nor_1 (Dec1_out[0], Dec1_in[0], Dec1_in[1], Dec1_in[2], Dec1_in[3]);
  nor nor_2 (Dec1_out[1], not_1_out[0], Dec1_in[1], Dec1_in[2], Dec1_in[3]);
  nor nor_3 (Dec1_out[2], Dec1_in[0], not_1_out[1], Dec1_in[2], Dec1_in[3]);
  nor nor_4 (Dec1_out[3], not_1_out[0], not_1_out[1], Dec1_in[2], Dec1_in[3]);
  nor nor_5 (Dec1_out[4], Dec1_in[0], Dec1_in[1], not_1_out[2], Dec1_in[3]);
  nor nor_6 (Dec1_out[5], not_1_out[0], Dec1_in[1], not_1_out[2], Dec1_in[3]);
  nor nor_7 (Dec1_out[6], Dec1_in[0], not_1_out[1], not_1_out[2], Dec1_in[3]);
  nor nor_8 (Dec1_out[7], not_1_out[0], not_1_out[1], not_1_out[2], Dec1_in[3]);
  nor nor_9 (Dec1_out[8], Dec1_in[0], Dec1_in[1], Dec1_in[2], not_1_out[3]);
  nor nor_10 (Dec1_out[9], not_1_out[0], Dec1_in[1], Dec1_in[2], not_1_out[3]);
  nor nor_11 (Dec1_out[10], Dec1_in[0], not_1_out[1], Dec1_in[2], not_1_out[3]);
  nor nor_12 (Dec1_out[11], not_1_out[0], not_1_out[1], Dec1_in[2], not_1_out[3]);
  nor nor_13 (Dec1_out[12], Dec1_in[0], Dec1_in[1], not_1_out[2], not_1_out[3]);
  nor nor_14 (Dec1_out[13], not_1_out[0], Dec1_in[1], not_1_out[2], not_1_out[3]);
  nor nor_15 (Dec1_out[14], Dec1_in[0], not_1_out[1], not_1_out[2], not_1_out[3]);
  nor nor_16 (Dec1_out[15], not_1_out[0], not_1_out[1], not_1_out[2], not_1_out[3]);
endmodule

module NOISE_Decoder2 (
  input  [15:0] Dec2_in,
  output [10:0] Dec2_out
);

  nor nor_1 (Dec2_out[0], Dec2_in[0], Dec2_in[1], Dec2_in[2], Dec2_in[9], Dec2_in[11], Dec2_in[12], Dec2_in[14], Dec2_in[15]);
  nor nor_2 (Dec2_out[1], Dec2_in[4], Dec2_in[8], Dec2_in[14], Dec2_in[15]);
  nor nor_3 (Dec2_out[2], Dec2_in[0], Dec2_in[1], Dec2_in[2], Dec2_in[3], Dec2_in[4], Dec2_in[5], Dec2_in[6], Dec2_in[8], Dec2_in[11], Dec2_in[12], Dec2_in[14], Dec2_in[15]);
  nor nor_4 (Dec2_out[3], Dec2_in[0], Dec2_in[5], Dec2_in[6], Dec2_in[7], Dec2_in[9], Dec2_in[10], Dec2_in[11], Dec2_in[12], Dec2_in[14], Dec2_in[15]);
  nor nor_5 (Dec2_out[4], Dec2_in[0], Dec2_in[1], Dec2_in[2], Dec2_in[6], Dec2_in[7], Dec2_in[8], Dec2_in[9], Dec2_in[10], Dec2_in[11], Dec2_in[12], Dec2_in[13], Dec2_in[14], Dec2_in[15]);
  nor nor_6 (Dec2_out[5], Dec2_in[0], Dec2_in[1], Dec2_in[9], Dec2_in[12], Dec2_in[13], Dec2_in[14], Dec2_in[15]);
  nor nor_7 (Dec2_out[6], Dec2_in[0], Dec2_in[1], Dec2_in[2], Dec2_in[3], Dec2_in[4], Dec2_in[8], Dec2_in[9], Dec2_in[10], Dec2_in[13], Dec2_in[14]);
  nor nor_8 (Dec2_out[7], Dec2_in[0], Dec2_in[1], Dec2_in[4], Dec2_in[5], Dec2_in[6], Dec2_in[7], Dec2_in[9], Dec2_in[10], Dec2_in[11], Dec2_in[12], Dec2_in[13], Dec2_in[14], Dec2_in[15]);
  nor nor_9 (Dec2_out[8], Dec2_in[0], Dec2_in[1], Dec2_in[2], Dec2_in[3], Dec2_in[6], Dec2_in[7], Dec2_in[10], Dec2_in[11], Dec2_in[12], Dec2_in[13]);
  nor nor_10 (Dec2_out[9], Dec2_in[0], Dec2_in[1], Dec2_in[2], Dec2_in[4], Dec2_in[5], Dec2_in[6], Dec2_in[7], Dec2_in[8], Dec2_in[9], Dec2_in[11], Dec2_in[15]);
  nor nor_11 (Dec2_out[10], Dec2_in[0], Dec2_in[1], Dec2_in[2], Dec2_in[3], Dec2_in[4], Dec2_in[5], Dec2_in[6], Dec2_in[7], Dec2_in[8], Dec2_in[9], Dec2_in[10], Dec2_in[11], Dec2_in[13], Dec2_in[14], Dec2_in[15]);
endmodule

module NOISE_FreqLFSR (
  input  ACLK,
  input  n_ACLK,
  input  RES,
  input  [10:0] NNF,
  output RSTEP
);

  wire and_1_out, nor_1_out, nor_2_out, nor_4_out, nor_5_out, nor_6_out, nor_7_out, not_1_out, not_2_out,
       not_3_out, not_4_out, not_5_out;
  wire [10:0] lsb_sout;

  not not_1 (not_1_out, ACLK);
  not not_2 (not_2_out, nor_5_out);
  FreqLFSRBit msb (
    .n_ACLK(n_ACLK), .load(RSTEP), .step(nor_4_out), .val(NNF[10]), .sin(nor_7_out), .sout(lsb_sout[10]));
  FreqLFSRBit freqlfsrbit_1 (
    .n_ACLK(n_ACLK), .load(RSTEP), .step(nor_4_out), .val(NNF[6]), .sin(lsb_sout[7]), .sout(lsb_sout[6]));
  FreqLFSRBit freqlfsrbit_2 (
    .n_ACLK(n_ACLK), .load(RSTEP), .step(nor_4_out), .val(NNF[2]), .sin(lsb_sout[3]), .sout(lsb_sout[2]));
  nor nor_1 (nor_1_out, lsb_sout[0], lsb_sout[1], lsb_sout[2], lsb_sout[3], lsb_sout[4], lsb_sout[5], lsb_sout[6], lsb_sout[7], lsb_sout[8], lsb_sout[9], lsb_sout[10]);
  not not_3 (not_3_out, not_1_out);
  nor nor_2 (nor_2_out, not_2_out, RES);
  not not_4 (not_4_out, nor_2_out);
  nor nor_3 (RSTEP, not_3_out, nor_2_out);
  nor nor_4 (nor_4_out, not_3_out, not_4_out);
  FreqLFSRBit freqlfsrbit_3 (
    .n_ACLK(n_ACLK), .load(RSTEP), .step(nor_4_out), .val(NNF[9]), .sin(lsb_sout[10]), .sout(lsb_sout[9]));
  FreqLFSRBit freqlfsrbit_4 (
    .n_ACLK(n_ACLK), .load(RSTEP), .step(nor_4_out), .val(NNF[5]), .sin(lsb_sout[6]), .sout(lsb_sout[5]));
  FreqLFSRBit freqlfsrbit_5 (
    .n_ACLK(n_ACLK), .load(RSTEP), .step(nor_4_out), .val(NNF[1]), .sin(lsb_sout[2]), .sout(lsb_sout[1]));
  not not_5 (not_5_out, lsb_sout[0]);
  nor nor_5 (nor_5_out, not_5_out, lsb_sout[1], lsb_sout[2], lsb_sout[3], lsb_sout[4], lsb_sout[5], lsb_sout[6], lsb_sout[7], lsb_sout[8], lsb_sout[9], lsb_sout[10]);
  FreqLFSRBit freqlfsrbit_6 (
    .n_ACLK(n_ACLK), .load(RSTEP), .step(nor_4_out), .val(NNF[8]), .sin(lsb_sout[9]), .sout(lsb_sout[8]));
  FreqLFSRBit freqlfsrbit_7 (
    .n_ACLK(n_ACLK), .load(RSTEP), .step(nor_4_out), .val(NNF[4]), .sin(lsb_sout[5]), .sout(lsb_sout[4]));
  FreqLFSRBit lsb (
    .n_ACLK(n_ACLK), .load(RSTEP), .step(nor_4_out), .val(NNF[0]), .sin(lsb_sout[1]), .sout(lsb_sout[0]));
  and and_1 (and_1_out, lsb_sout[0], lsb_sout[2]);
  nor nor_6 (nor_6_out, lsb_sout[0], lsb_sout[2], nor_1_out);
  FreqLFSRBit freqlfsrbit_8 (
    .n_ACLK(n_ACLK), .load(RSTEP), .step(nor_4_out), .val(NNF[7]), .sin(lsb_sout[8]), .sout(lsb_sout[7]));
  FreqLFSRBit freqlfsrbit_9 (
    .n_ACLK(n_ACLK), .load(RSTEP), .step(nor_4_out), .val(NNF[3]), .sin(lsb_sout[4]), .sout(lsb_sout[3]));
  nor nor_7 (nor_7_out, and_1_out, nor_6_out, RES);

  // Notes on the sheet:
  //   /ACLK4
  //   NFZ
  //   NFLOAD
  //   NFSTEP
  //   NFOUT
  //   NSIN
endmodule

module NOISE_RandomLFSR (
  input  n_ACLK,
  input  RSTEP,
  input  NORND,
  input  LOCK,
  input  W400E,
  input  [7:0] DB_in,
  output RNDOUT
);

  wire and_1_out, multiplexer_1_out, nor_1_out, nor_2_out, nor_3_out, nor_5_out, rmod_reg_n_valout,
       rmod_reg_valout;
  wire [14:0] lsb_sout;

  RandomLFSRBit msb (.n_ACLK(n_ACLK), .load(RSTEP), .sin(nor_3_out), .sout(lsb_sout[14]));
  RandomLFSRBit randomlfsrbit_1 (.n_ACLK(n_ACLK), .load(RSTEP), .sin(lsb_sout[11]), .sout(lsb_sout[10]));
  RandomLFSRBit randomlfsrbit_2 (.n_ACLK(n_ACLK), .load(RSTEP), .sin(lsb_sout[7]), .sout(lsb_sout[6]));
  RandomLFSRBit randomlfsrbit_3 (.n_ACLK(n_ACLK), .load(RSTEP), .sin(lsb_sout[3]), .sout(lsb_sout[2]));
  RegisterBit rmod_reg (
    .n_ACLK(n_ACLK), .Enable(W400E), .Value(DB_in[7]), .ValOut(rmod_reg_valout), .n_ValOut(rmod_reg_n_valout));
  // NoConnect on rmod_reg_n_valout
  Multiplexer multiplexer_1 (.in0(lsb_sout[1]), .in1(lsb_sout[6]), .out(multiplexer_1_out), .sel(rmod_reg_valout));
  RandomLFSRBit randomlfsrbit_4 (.n_ACLK(n_ACLK), .load(RSTEP), .sin(lsb_sout[14]), .sout(lsb_sout[13]));
  RandomLFSRBit randomlfsrbit_5 (.n_ACLK(n_ACLK), .load(RSTEP), .sin(lsb_sout[10]), .sout(lsb_sout[9]));
  RandomLFSRBit randomlfsrbit_6 (.n_ACLK(n_ACLK), .load(RSTEP), .sin(lsb_sout[6]), .sout(lsb_sout[5]));
  RandomLFSRBit randomlfsrbit_7 (.n_ACLK(n_ACLK), .load(RSTEP), .sin(lsb_sout[2]), .sout(lsb_sout[1]));
  nor nor_1 (nor_1_out, nor_5_out, lsb_sout[0], multiplexer_1_out);
  and and_1 (and_1_out, lsb_sout[0], multiplexer_1_out);
  RandomLFSRBit randomlfsrbit_8 (.n_ACLK(n_ACLK), .load(RSTEP), .sin(lsb_sout[13]), .sout(lsb_sout[12]));
  RandomLFSRBit randomlfsrbit_9 (.n_ACLK(n_ACLK), .load(RSTEP), .sin(lsb_sout[9]), .sout(lsb_sout[8]));
  RandomLFSRBit randomlfsrbit_10 (.n_ACLK(n_ACLK), .load(RSTEP), .sin(lsb_sout[5]), .sout(lsb_sout[4]));
  RandomLFSRBit lsb (.n_ACLK(n_ACLK), .load(RSTEP), .sin(lsb_sout[1]), .sout(lsb_sout[0]));
  nor nor_2 (nor_2_out, lsb_sout[0], NORND);
  nor nor_3 (nor_3_out, LOCK, nor_1_out, and_1_out);
  RandomLFSRBit randomlfsrbit_11 (.n_ACLK(n_ACLK), .load(RSTEP), .sin(lsb_sout[12]), .sout(lsb_sout[11]));
  RandomLFSRBit randomlfsrbit_12 (.n_ACLK(n_ACLK), .load(RSTEP), .sin(lsb_sout[8]), .sout(lsb_sout[7]));
  RandomLFSRBit randomlfsrbit_13 (.n_ACLK(n_ACLK), .load(RSTEP), .sin(lsb_sout[4]), .sout(lsb_sout[3]));
  nor nor_4 (RNDOUT, nor_2_out, LOCK);
  nor nor_5 (nor_5_out, lsb_sout[0], lsb_sout[1], lsb_sout[2], lsb_sout[3], lsb_sout[4], lsb_sout[5], lsb_sout[6], lsb_sout[7], lsb_sout[8], lsb_sout[9], lsb_sout[10], lsb_sout[11], lsb_sout[12], lsb_sout[13], lsb_sout[14]);

  // Notes on the sheet:
  //   RIN
  //   RSOZ
endmodule

module FreqLFSRBit (
  input  n_ACLK,
  input  load,
  input  step,
  input  val,
  input  sin,
  output sout
);

  wire controlled_buffer_1_out, in_latch_nq;

  assign controlled_buffer_1_out = load ? val : 1'bz;  // Controlled_Buffer controlled_buffer_1
  assign controlled_buffer_1_out = step ? sin : 1'bz;  // Controlled_Buffer controlled_buffer_2
  TranspDLatch in_latch (.d(controlled_buffer_1_out), .nq(in_latch_nq));  // open: q
  DLatch out_latch (.Enable(n_ACLK), .Value(in_latch_nq), .n_ValOut(sout));  // open: ValOut
endmodule

module RandomLFSRBit (
  input  n_ACLK,
  input  load,
  input  sin,
  output sout
);

  wire in_reg_n_valout;

  RegisterBit in_reg (.n_ACLK(n_ACLK), .Enable(load), .Value(sin), .n_ValOut(in_reg_n_valout));  // open: ValOut
  DLatch out_latch (.Enable(n_ACLK), .Value(in_reg_n_valout), .n_ValOut(sout));  // open: ValOut
endmodule
