// Logisim project NMOS_CheatSheet.circ as structural Verilog
module PlexedTranspLatch (
  input  sel_A,
  input  A,
  input  sel_B,
  input  B,
  input  sel_C,
  input  C,
  output n_val_out,
  output value_out,
  output n_value_out
);

  wire multiplexer_1_out, multiplexer_2_out, multiplexer_3_out, transistor_1_out, undriven;

  Transistor #(.\type ("n")) transistor_1 (.in(A), .out(transistor_1_out), .gate(sel_A));
  Transistor #(.\type ("n")) transistor_2 (.in(B), .out(transistor_1_out), .gate(sel_B));
  // NoConnect on undriven
  Multiplexer multiplexer_1 (.in0(undriven), .in1(A), .out(multiplexer_1_out), .sel(sel_A));
  Transistor #(.\type ("n")) transistor_3 (.in(C), .out(transistor_1_out), .gate(sel_C));
  Multiplexer multiplexer_2 (.in0(multiplexer_1_out), .in1(B), .out(multiplexer_2_out), .sel(sel_B));
  Multiplexer multiplexer_3 (.in0(multiplexer_2_out), .in1(C), .out(multiplexer_3_out), .sel(sel_C));
  Transistor #(.\type ("n")) transistor_4 (.in(1'b0), .out(n_val_out), .gate(transistor_1_out));
  D_Flip_Flop #(.trigger("high")) d_ff_1 (
    .D(multiplexer_3_out), .clk(1'b1), .Q(value_out), .Qn(n_value_out));  // open: preset, reset

  // Notes on the sheet:
  //   Transparent Latch
  //   Transparent Latch
endmodule

module AOI (
  input  in_1,
  input  in_2,
  input  in_3,
  output out_4
);

  wire and_1_out, transistor_1_out;

  Pull_Resistor #(.pull(1)) pull_resistor_1 (.node(out_4));
  Transistor #(.\type ("n")) transistor_1 (.in(1'b0), .out(transistor_1_out), .gate(in_1));
  Transistor #(.\type ("n")) transistor_2 (.in(transistor_1_out), .out(out_4), .gate(in_2));
  and and_1 (and_1_out, in_1, in_2);
  Transistor #(.\type ("n")) transistor_3 (.in(1'b0), .out(out_4), .gate(in_3));
  nor nor_1 (out_4, and_1_out, in_3);

  // Other names for the same wires on the sheet: a = in_1; b = in_2; c = in_3; x = out_4
endmodule

module OAI (
  input  in_1,
  input  in_2,
  input  in_3,
  output out_4
);

  wire or_1_out, transistor_1_out;

  Transistor #(.\type ("n")) transistor_1 (.in(1'b0), .out(transistor_1_out), .gate(in_1));
  Transistor #(.\type ("n")) transistor_2 (.in(1'b0), .out(transistor_1_out), .gate(in_2));
  or or_1 (or_1_out, in_1, in_2);
  Transistor #(.\type ("n")) transistor_3 (.in(transistor_1_out), .out(out_4), .gate(in_3));
  Pull_Resistor #(.pull(1)) pull_resistor_1 (.node(out_4));
  nand nand_1 (out_4, or_1_out, in_3);

  // Other names for the same wires on the sheet: a = in_1; b = in_2; c = in_3; x = out_4
endmodule
