// Logisim project 2C02_PPU.circ as structural Verilog
module _2C02_PPU (
  input  EXT3,
  input  EXT2,
  input  EXT1,
  input  EXT0,
  input  nDBE,
  input  RS0,
  input  RS1,
  input  RS2,
  input  D7,
  input  D6,
  input  D5,
  input  D4,
  input  D3,
  input  D2,
  input  D1,
  input  D0,
  input  R_W,
  input  nRES,
  input  in_19,
  input  in_20,
  input  in_21,
  input  in_22,
  input  in_23,
  input  in_24,
  input  in_25,
  input  in_26,
  input  in_27,
  output nINT,
  output [10:0] VOUT,
  output nWR,
  output nRD,
  output A13,
  output A12,
  output A11,
  output A10,
  output A9,
  output A8
);

  wire CLK_out, cpu_data_pad_1_db_in, h_counter_1_h0, h_counter_1_h1, h_counter_1_h2, h_counter_1_h3,
       h_counter_1_h4, h_counter_1_h5, h_counter_1_h6, h_counter_1_h7, h_counter_1_h8, hv_select_1__0,
       hv_select_1__0_1, hv_select_1__0_7a, hv_select_1__0_7b, hv_select_1__0_63, hv_select_1__0_255,
       hv_select_1__2_3, hv_select_1__4_5, hv_select_1__6_7, hv_select_1__63, hv_select_1__65,
       hv_select_1__240, hv_select_1__241, hv_select_1__241_2, hv_select_1__244, hv_select_1__247,
       hv_select_1__255, hv_select_1__256, hv_select_1__256_319, hv_select_1__261, hv_select_1__261_2,
       hv_select_1__261_3, hv_select_1__270, hv_select_1__279, hv_select_1__279_2, hv_select_1__304,
       hv_select_1__308, hv_select_1__323, hv_select_1__328, hv_select_1__335_339, hv_select_1__336_340a,
       hv_select_1__336_340b, hv_select_1__340, pixel_clock_1_pclk, reset_ff_1_res, undriven, v_counter_1_v0,
       v_counter_1_v1, v_counter_1_v2, v_counter_1_v3, v_counter_1_v4, v_counter_1_v5, v_counter_1_v6,
       v_counter_1_v7, v_counter_1_v8;

  Clock CLK (.out(CLK_out));
  PIXEL_CLOCK pixel_clock_1 (.CLK(CLK_out), .RES(reset_ff_1_res), .PCLK(pixel_clock_1_pclk));
  RESET_FF reset_ff_1 (.nRES(nRES), .RES(reset_ff_1_res));  // open: RESCL, RC
  VIDEO_OUT video_out_1 (
    .CLK(CLK_out), .RES(reset_ff_1_res), .nTR(1'b1), .nTG(1'b1), .nTB(1'b1), .PCLK(pixel_clock_1_pclk),
    .CC0(in_25), .CC1(in_24), .CC2(in_23), .CC3(in_22), .SYNC(in_19), .BURST(in_20), .PICTURE(in_21),
    .LL0(in_27), .LL1(in_26), .out_16(VOUT));
  HV_SELECT hv_select_1 (
    .H8(h_counter_1_h8), .H7(h_counter_1_h7), .H6(h_counter_1_h6), .H5(h_counter_1_h5), .H4(h_counter_1_h4),
    .H3(h_counter_1_h3), .H2(h_counter_1_h2), .H1(h_counter_1_h1), .H0(h_counter_1_h0), .VB(1'b0),
    .BLNK(1'b0), ._279(hv_select_1__279), ._256(hv_select_1__256), ._65(hv_select_1__65),
    ._0_7A(hv_select_1__0_7a), ._0_7B(hv_select_1__0_7b), ._335_339(hv_select_1__335_339),
    ._63(hv_select_1__63), ._255(hv_select_1__255), ._0_63(hv_select_1__0_63),
    ._256_319(hv_select_1__256_319), ._0_255(hv_select_1__0_255), ._0_1(hv_select_1__0_1),
    ._6_7(hv_select_1__6_7), ._4_5(hv_select_1__4_5), ._336_340A(hv_select_1__336_340a),
    ._336_340B(hv_select_1__336_340b), ._2_3(hv_select_1__2_3), ._270(hv_select_1__270),
    ._328(hv_select_1__328), ._279_2(hv_select_1__279_2), ._304(hv_select_1__304), ._323(hv_select_1__323),
    ._308(hv_select_1__308), ._340(hv_select_1__340), ._247(hv_select_1__247), .V8(v_counter_1_v8),
    .V7(v_counter_1_v7), .V6(v_counter_1_v6), .V5(v_counter_1_v5), .V4(v_counter_1_v4), .V3(v_counter_1_v3),
    .V2(v_counter_1_v2), .V1(v_counter_1_v1), .V0(v_counter_1_v0), ._244(hv_select_1__244),
    ._261(hv_select_1__261), ._241(hv_select_1__241), ._241_2(hv_select_1__241_2), ._0(hv_select_1__0),
    ._240(hv_select_1__240), ._261_2(hv_select_1__261_2), ._261_3(hv_select_1__261_3));
  H_COUNTER h_counter_1 (
    .HC(1'b0), .RES(reset_ff_1_res), .CLK(pixel_clock_1_pclk), .H0(h_counter_1_h0), .H1(h_counter_1_h1),
    .H2(h_counter_1_h2), .H3(h_counter_1_h3), .H4(h_counter_1_h4), .H5(h_counter_1_h5), .H6(h_counter_1_h6),
    .H7(h_counter_1_h7), .H8(h_counter_1_h8));
  V_COUNTER v_counter_1 (
    .VC(1'b0), .RES(reset_ff_1_res), .CLK(pixel_clock_1_pclk), .V0(v_counter_1_v0), .V1(v_counter_1_v1),
    .V2(v_counter_1_v2), .V3(v_counter_1_v3), .V4(v_counter_1_v4), .V5(v_counter_1_v5), .V6(v_counter_1_v6),
    .V7(v_counter_1_v7), .V8(v_counter_1_v8), .VIN(1'b0));
  REGISTER_SELECT register_select_1 ();  // open: nDBE, RC, RS0, RS1, RS2, R_W, nW6_1, nW6_2, nW5_1, nW5_2, nR7, nW7, nW4, nW3, nR2, nW1, nW0, nR4
  CPU_DATA_PAD cpu_data_pad_1 (.DB_out(undriven), .DB_in(cpu_data_pad_1_db_in));  // open: WR, RD, PPU_DATA, DATA_PPU

  // Notes on the sheet:
  //   VRAM INTERFACE
  //   CPU INTERFACE
endmodule

module D_latch (
  input  EN,
  input  D,
  output Q,
  output NOT_Q
);

  D_Flip_Flop #(.trigger("high")) d_ff_1 (.clk(EN), .D(D), .Q(Q), .Qn(NOT_Q));  // open: preset, en, reset
endmodule

module PIXEL_CLOCK (
  input  CLK,
  input  RES,
  output PCLK
);

  wire d_latch_1_not_q, d_latch_2_not_q, d_latch_3_not_q, nor_1_out, not_1_out;

  not not_1 (not_1_out, CLK);
  nor nor_1 (nor_1_out, RES, PCLK);
  D_latch d_latch_1 (.EN(CLK), .D(nor_1_out), .NOT_Q(d_latch_1_not_q));  // open: Q
  D_latch d_latch_2 (.EN(not_1_out), .D(d_latch_1_not_q), .NOT_Q(d_latch_2_not_q));  // open: Q
  D_latch d_latch_3 (.EN(CLK), .D(d_latch_2_not_q), .NOT_Q(d_latch_3_not_q));  // open: Q
  D_latch d_latch_4 (.EN(not_1_out), .D(d_latch_3_not_q), .NOT_Q(PCLK));  // open: Q

  // Notes on the sheet:
  //   Pixel clock is disabled during RESET (PPU stall)
  //   PCLK = CLK / 4
endmodule

module RESET_FF (
  input  nRES,
  input  RESCL,
  output RES,
  output RC
);

  wire nor_1_out;

  not not_1 (RES, nRES);
  nor nor_1 (nor_1_out, RES, RC);
  nor nor_2 (RC, nor_1_out, RESCL);

  // Notes on the sheet:
  //   Reset flip/flop remains set after RESET, until not cleared by RESCL
  //   Reset flip/flop
  //   (REG CLEAR)
endmodule

module COUNTER_BIT (
  input  in,
  input  CLK,
  input  clear,
  input  RES,
  output value
);

  wire d_latch_1_q, multiplexer_1_out, multiplexer_2_out, nor_2_out, not_1_out, not_2_out;

  not not_1 (not_1_out, CLK);
  Multiplexer multiplexer_1 (.in0(not_2_out), .in1(value), .out(multiplexer_1_out), .sel(in));  // open: en
  not not_2 (not_2_out, multiplexer_2_out);
  Multiplexer multiplexer_2 (.in0(value), .in1(nor_2_out), .out(multiplexer_2_out), .sel(CLK));  // open: en
  nor nor_1 (value, not_2_out, RES);
  nor nor_2 (nor_2_out, d_latch_1_q, clear);
  D_latch d_latch_1 (.EN(not_1_out), .D(multiplexer_1_out), .Q(d_latch_1_q));  // open: NOT_Q

  // Notes on the sheet:
  //   carry_in
  //   clear manually
  //   global RESET
  //   carry_out
endmodule

module H_COUNTER (
  input  HC,
  input  RES,
  input  CLK,
  output H0,
  output H1,
  output H2,
  output H3,
  output H4,
  output H5,
  output H6,
  output H7,
  output H8
);

  wire and_1_out, and_2_out, and_3_out, and_4_out, and_5_out, and_6_out, and_7_out, and_8_out;

  COUNTER_BIT counter_bit_1 (.in(1'b1), .CLK(CLK), .clear(HC), .RES(RES), .value(H0));
  and and_1 (and_1_out, H0, 1'b1);
  COUNTER_BIT counter_bit_2 (.in(and_1_out), .CLK(CLK), .clear(HC), .RES(RES), .value(H1));
  and and_2 (and_2_out, H1, and_1_out);
  COUNTER_BIT counter_bit_3 (.in(and_2_out), .CLK(CLK), .clear(HC), .RES(RES), .value(H2));
  and and_3 (and_3_out, H2, and_2_out);
  COUNTER_BIT counter_bit_4 (.in(and_3_out), .CLK(CLK), .clear(HC), .RES(RES), .value(H3));
  and and_4 (and_4_out, H3, and_3_out);
  COUNTER_BIT counter_bit_5 (.in(and_4_out), .CLK(CLK), .clear(HC), .RES(RES), .value(H4));
  and and_5 (and_5_out, H4, H3, H2, H1, H0);
  COUNTER_BIT counter_bit_6 (.in(and_5_out), .CLK(CLK), .clear(HC), .RES(RES), .value(H5));
  and and_6 (and_6_out, H5, and_5_out);
  COUNTER_BIT counter_bit_7 (.in(and_6_out), .CLK(CLK), .clear(HC), .RES(RES), .value(H6));
  and and_7 (and_7_out, H6, and_6_out);
  COUNTER_BIT counter_bit_8 (.in(and_7_out), .CLK(CLK), .clear(HC), .RES(RES), .value(H7));
  and and_8 (and_8_out, H7, and_7_out);
  COUNTER_BIT counter_bit_9 (.in(and_8_out), .CLK(CLK), .clear(HC), .RES(RES), .value(H8));

  // Notes on the sheet:
  //   reduce propagation delay
endmodule

module V_COUNTER (
  input  VC,
  input  RES,
  input  CLK,
  input  VIN,
  output V0,
  output V1,
  output V2,
  output V3,
  output V4,
  output V5,
  output V6,
  output V7,
  output V8
);

  wire and_1_out, and_2_out, and_3_out, and_4_out, and_5_out, and_6_out, and_7_out, and_8_out;

  COUNTER_BIT counter_bit_1 (.in(VIN), .CLK(CLK), .clear(VC), .RES(RES), .value(V0));
  and and_1 (and_1_out, V0, VIN);
  COUNTER_BIT counter_bit_2 (.in(and_1_out), .CLK(CLK), .clear(VC), .RES(RES), .value(V1));
  and and_2 (and_2_out, V1, and_1_out);
  COUNTER_BIT counter_bit_3 (.in(and_2_out), .CLK(CLK), .clear(VC), .RES(RES), .value(V2));
  and and_3 (and_3_out, V2, and_2_out);
  COUNTER_BIT counter_bit_4 (.in(and_3_out), .CLK(CLK), .clear(VC), .RES(RES), .value(V3));
  and and_4 (and_4_out, V3, and_3_out);
  COUNTER_BIT counter_bit_5 (.in(and_4_out), .CLK(CLK), .clear(VC), .RES(RES), .value(V4));
  and and_5 (and_5_out, V4, V3, V2, V1, V0);
  COUNTER_BIT counter_bit_6 (.in(and_5_out), .CLK(CLK), .clear(VC), .RES(RES), .value(V5));
  and and_6 (and_6_out, V5, and_5_out);
  COUNTER_BIT counter_bit_7 (.in(and_6_out), .CLK(CLK), .clear(VC), .RES(RES), .value(V6));
  and and_7 (and_7_out, V6, and_6_out);
  COUNTER_BIT counter_bit_8 (.in(and_7_out), .CLK(CLK), .clear(VC), .RES(RES), .value(V7));
  and and_8 (and_8_out, V7, and_7_out);
  COUNTER_BIT counter_bit_9 (.in(and_8_out), .CLK(CLK), .clear(VC), .RES(RES), .value(V8));

  // Notes on the sheet:
  //   reduce propagation delay
endmodule

module HV_SELECT (
  input  H8,
  input  H7,
  input  H6,
  input  H5,
  input  H4,
  input  H3,
  input  H2,
  input  H1,
  input  H0,
  input  VB,
  input  BLNK,
  input  V8,
  input  V7,
  input  V6,
  input  V5,
  input  V4,
  input  V3,
  input  V2,
  input  V1,
  input  V0,
  output _279,
  output _256,
  output _65,
  output _0_7A,
  output _0_7B,
  output _335_339,
  output _63,
  output _255,
  output _0_63,
  output _256_319,
  output _0_255,
  output _0_1,
  output _6_7,
  output _4_5,
  output _336_340A,
  output _336_340B,
  output _2_3,
  output _270,
  output _328,
  output _279_2,
  output _304,
  output _323,
  output _308,
  output _340,
  output _247,
  output _244,
  output _261,
  output _241,
  output _241_2,
  output _0,
  output _240,
  output _261_2,
  output _261_3
);

  wire not_1_out, not_2_out, not_3_out, not_4_out, not_5_out, not_6_out, not_7_out, not_8_out, not_9_out,
       not_10_out, not_11_out, not_12_out, not_13_out, not_14_out, not_15_out, not_16_out, not_17_out,
       not_18_out;

  not not_1 (not_1_out, H8);
  not not_2 (not_2_out, H7);
  not not_3 (not_3_out, H6);
  not not_4 (not_4_out, H5);
  not not_5 (not_5_out, H4);
  not not_6 (not_6_out, H3);
  not not_7 (not_7_out, H2);
  not not_8 (not_8_out, H1);
  not not_9 (not_9_out, H0);
  not not_10 (not_10_out, V8);
  not not_11 (not_11_out, V7);
  not not_12 (not_12_out, V6);
  not not_13 (not_13_out, V5);
  not not_14 (not_14_out, V4);
  not not_15 (not_15_out, V3);
  not not_16 (not_16_out, V2);
  not not_17 (not_17_out, V1);
  not not_18 (not_18_out, V0);
  Pull_Resistor #(.pull(1)) pull_resistor_1 (.node(_279));
  Transistor #(.\type ("n")) transistor_1 (.in(1'b0), .out(_279), .gate(not_1_out));
  Transistor #(.\type ("n")) transistor_2 (.in(1'b0), .out(_279), .gate(H7));
  Transistor #(.\type ("n")) transistor_3 (.in(1'b0), .out(_279), .gate(H6));
  Transistor #(.\type ("n")) transistor_4 (.in(1'b0), .out(_279), .gate(H5));
  Transistor #(.\type ("n")) transistor_5 (.in(1'b0), .out(_279), .gate(not_5_out));
  Transistor #(.\type ("n")) transistor_6 (.in(1'b0), .out(_279), .gate(H3));
  Transistor #(.\type ("n")) transistor_7 (.in(1'b0), .out(_279), .gate(not_7_out));
  Transistor #(.\type ("n")) transistor_8 (.in(1'b0), .out(_279), .gate(not_8_out));
  Transistor #(.\type ("n")) transistor_9 (.in(1'b0), .out(_279), .gate(not_9_out));
  Pull_Resistor #(.pull(1)) pull_resistor_2 (.node(_247));
  Transistor #(.\type ("n")) transistor_10 (.in(1'b0), .out(_247), .gate(not_11_out));
  Transistor #(.\type ("n")) transistor_11 (.in(1'b0), .out(_247), .gate(not_12_out));
  Transistor #(.\type ("n")) transistor_12 (.in(1'b0), .out(_247), .gate(V4));
  Transistor #(.\type ("n")) transistor_13 (.in(1'b0), .out(_247), .gate(not_14_out));
  Transistor #(.\type ("n")) transistor_14 (.in(1'b0), .out(_247), .gate(V3));
  Transistor #(.\type ("n")) transistor_15 (.in(1'b0), .out(_247), .gate(not_16_out));
  Transistor #(.\type ("n")) transistor_16 (.in(1'b0), .out(_247), .gate(not_17_out));
  Transistor #(.\type ("n")) transistor_17 (.in(1'b0), .out(_247), .gate(not_18_out));
  Pull_Resistor #(.pull(1)) pull_resistor_3 (.node(_256));
  Transistor #(.\type ("n")) transistor_18 (.in(1'b0), .out(_256), .gate(not_1_out));
  Transistor #(.\type ("n")) transistor_19 (.in(1'b0), .out(_256), .gate(H7));
  Transistor #(.\type ("n")) transistor_20 (.in(1'b0), .out(_256), .gate(H6));
  Transistor #(.\type ("n")) transistor_21 (.in(1'b0), .out(_256), .gate(H5));
  Transistor #(.\type ("n")) transistor_22 (.in(1'b0), .out(_256), .gate(H4));
  Transistor #(.\type ("n")) transistor_23 (.in(1'b0), .out(_256), .gate(H3));
  Transistor #(.\type ("n")) transistor_24 (.in(1'b0), .out(_256), .gate(H2));
  Transistor #(.\type ("n")) transistor_25 (.in(1'b0), .out(_256), .gate(H1));
  Transistor #(.\type ("n")) transistor_26 (.in(1'b0), .out(_256), .gate(H0));
  Pull_Resistor #(.pull(1)) pull_resistor_4 (.node(_244));
  Transistor #(.\type ("n")) transistor_27 (.in(1'b0), .out(_244), .gate(not_11_out));
  Transistor #(.\type ("n")) transistor_28 (.in(1'b0), .out(_244), .gate(not_12_out));
  Transistor #(.\type ("n")) transistor_29 (.in(1'b0), .out(_244), .gate(not_13_out));
  Transistor #(.\type ("n")) transistor_30 (.in(1'b0), .out(_244), .gate(not_14_out));
  Transistor #(.\type ("n")) transistor_31 (.in(1'b0), .out(_244), .gate(V3));
  Transistor #(.\type ("n")) transistor_32 (.in(1'b0), .out(_244), .gate(not_16_out));
  Transistor #(.\type ("n")) transistor_33 (.in(1'b0), .out(_244), .gate(V1));
  Transistor #(.\type ("n")) transistor_34 (.in(1'b0), .out(_244), .gate(V0));
  Pull_Resistor #(.pull(1)) pull_resistor_5 (.node(_65));
  Transistor #(.\type ("n")) transistor_35 (.in(1'b0), .out(_65), .gate(H8));
  Transistor #(.\type ("n")) transistor_36 (.in(1'b0), .out(_65), .gate(H7));
  Transistor #(.\type ("n")) transistor_37 (.in(1'b0), .out(_65), .gate(not_3_out));
  Transistor #(.\type ("n")) transistor_38 (.in(1'b0), .out(_65), .gate(H5));
  Transistor #(.\type ("n")) transistor_39 (.in(1'b0), .out(_65), .gate(H4));
  Transistor #(.\type ("n")) transistor_40 (.in(1'b0), .out(_65), .gate(H3));
  Transistor #(.\type ("n")) transistor_41 (.in(1'b0), .out(_65), .gate(H2));
  Transistor #(.\type ("n")) transistor_42 (.in(1'b0), .out(_65), .gate(H1));
  Transistor #(.\type ("n")) transistor_43 (.in(1'b0), .out(_65), .gate(not_9_out));
  Transistor #(.\type ("n")) transistor_44 (.in(1'b0), .out(_65), .gate(BLNK));
  Pull_Resistor #(.pull(1)) pull_resistor_6 (.node(_261));
  Transistor #(.\type ("n")) transistor_45 (.in(1'b0), .out(_261), .gate(not_10_out));
  Transistor #(.\type ("n")) transistor_46 (.in(1'b0), .out(_261), .gate(V7));
  Transistor #(.\type ("n")) transistor_47 (.in(1'b0), .out(_261), .gate(V6));
  Transistor #(.\type ("n")) transistor_48 (.in(1'b0), .out(_261), .gate(V5));
  Transistor #(.\type ("n")) transistor_49 (.in(1'b0), .out(_261), .gate(V4));
  Transistor #(.\type ("n")) transistor_50 (.in(1'b0), .out(_261), .gate(V3));
  Transistor #(.\type ("n")) transistor_51 (.in(1'b0), .out(_261), .gate(not_16_out));
  Transistor #(.\type ("n")) transistor_52 (.in(1'b0), .out(_261), .gate(V1));
  Transistor #(.\type ("n")) transistor_53 (.in(1'b0), .out(_261), .gate(not_18_out));
  Pull_Resistor #(.pull(1)) pull_resistor_7 (.node(_0_7A));
  Transistor #(.\type ("n")) transistor_54 (.in(1'b0), .out(_0_7A), .gate(H7));
  Transistor #(.\type ("n")) transistor_55 (.in(1'b0), .out(_0_7A), .gate(H6));
  Transistor #(.\type ("n")) transistor_56 (.in(1'b0), .out(_0_7A), .gate(H5));
  Transistor #(.\type ("n")) transistor_57 (.in(1'b0), .out(_0_7A), .gate(H4));
  Transistor #(.\type ("n")) transistor_58 (.in(1'b0), .out(_0_7A), .gate(H3));
  Pull_Resistor #(.pull(1)) pull_resistor_8 (.node(_241));
  Transistor #(.\type ("n")) transistor_59 (.in(1'b0), .out(_241), .gate(not_11_out));
  Transistor #(.\type ("n")) transistor_60 (.in(1'b0), .out(_241), .gate(not_12_out));
  Transistor #(.\type ("n")) transistor_61 (.in(1'b0), .out(_241), .gate(not_13_out));
  Transistor #(.\type ("n")) transistor_62 (.in(1'b0), .out(_241), .gate(not_14_out));
  Transistor #(.\type ("n")) transistor_63 (.in(1'b0), .out(_241), .gate(V3));
  Transistor #(.\type ("n")) transistor_64 (.in(1'b0), .out(_241), .gate(V2));
  Transistor #(.\type ("n")) transistor_65 (.in(1'b0), .out(_241), .gate(V1));
  Transistor #(.\type ("n")) transistor_66 (.in(1'b0), .out(_241), .gate(not_18_out));
  Pull_Resistor #(.pull(1)) pull_resistor_9 (.node(_0_7B));
  Pull_Resistor #(.pull(1)) pull_resistor_10 (.node(_335_339));
  Transistor #(.\type ("n")) transistor_67 (.in(1'b0), .out(_0_7B), .gate(H8));
  Transistor #(.\type ("n")) transistor_68 (.in(1'b0), .out(_335_339), .gate(not_1_out));
  Transistor #(.\type ("n")) transistor_69 (.in(1'b0), .out(_335_339), .gate(H7));
  Transistor #(.\type ("n")) transistor_70 (.in(1'b0), .out(_335_339), .gate(not_3_out));
  Transistor #(.\type ("n")) transistor_71 (.in(1'b0), .out(_335_339), .gate(H5));
  Transistor #(.\type ("n")) transistor_72 (.in(1'b0), .out(_335_339), .gate(not_5_out));
  Transistor #(.\type ("n")) transistor_73 (.in(1'b0), .out(_335_339), .gate(H3));
  Transistor #(.\type ("n")) transistor_74 (.in(1'b0), .out(_335_339), .gate(H2));
  Transistor #(.\type ("n")) transistor_75 (.in(1'b0), .out(_0_7B), .gate(VB));
  Pull_Resistor #(.pull(1)) pull_resistor_11 (.node(_0));
  Pull_Resistor #(.pull(1)) pull_resistor_12 (.node(_241_2));
  Transistor #(.\type ("n")) transistor_76 (.in(1'b0), .out(_0), .gate(V8));
  Transistor #(.\type ("n")) transistor_77 (.in(1'b0), .out(_0), .gate(V7));
  Transistor #(.\type ("n")) transistor_78 (.in(1'b0), .out(_241_2), .gate(not_11_out));
  Transistor #(.\type ("n")) transistor_79 (.in(1'b0), .out(_0), .gate(V6));
  Transistor #(.\type ("n")) transistor_80 (.in(1'b0), .out(_241_2), .gate(not_12_out));
  Transistor #(.\type ("n")) transistor_81 (.in(1'b0), .out(_0), .gate(V5));
  Transistor #(.\type ("n")) transistor_82 (.in(1'b0), .out(_241_2), .gate(not_13_out));
  Transistor #(.\type ("n")) transistor_83 (.in(1'b0), .out(_0), .gate(V4));
  Transistor #(.\type ("n")) transistor_84 (.in(1'b0), .out(_241_2), .gate(not_14_out));
  Transistor #(.\type ("n")) transistor_85 (.in(1'b0), .out(_241_2), .gate(V3));
  Transistor #(.\type ("n")) transistor_86 (.in(1'b0), .out(_0), .gate(V3));
  Transistor #(.\type ("n")) transistor_87 (.in(1'b0), .out(_241_2), .gate(V2));
  Transistor #(.\type ("n")) transistor_88 (.in(1'b0), .out(_0), .gate(V2));
  Transistor #(.\type ("n")) transistor_89 (.in(1'b0), .out(_0), .gate(V1));
  Transistor #(.\type ("n")) transistor_90 (.in(1'b0), .out(_241_2), .gate(V1));
  Transistor #(.\type ("n")) transistor_91 (.in(1'b0), .out(_0), .gate(V0));
  Transistor #(.\type ("n")) transistor_92 (.in(1'b0), .out(_241_2), .gate(not_18_out));
  Pull_Resistor #(.pull(1)) pull_resistor_13 (.node(_63));
  Transistor #(.\type ("n")) transistor_93 (.in(1'b0), .out(_63), .gate(H8));
  Transistor #(.\type ("n")) transistor_94 (.in(1'b0), .out(_63), .gate(H7));
  Transistor #(.\type ("n")) transistor_95 (.in(1'b0), .out(_63), .gate(H6));
  Transistor #(.\type ("n")) transistor_96 (.in(1'b0), .out(_63), .gate(not_4_out));
  Transistor #(.\type ("n")) transistor_97 (.in(1'b0), .out(_63), .gate(not_5_out));
  Transistor #(.\type ("n")) transistor_98 (.in(1'b0), .out(_63), .gate(not_6_out));
  Transistor #(.\type ("n")) transistor_99 (.in(1'b0), .out(_63), .gate(not_7_out));
  Transistor #(.\type ("n")) transistor_100 (.in(1'b0), .out(_63), .gate(not_8_out));
  Transistor #(.\type ("n")) transistor_101 (.in(1'b0), .out(_63), .gate(not_9_out));
  Pull_Resistor #(.pull(1)) pull_resistor_14 (.node(_240));
  Transistor #(.\type ("n")) transistor_102 (.in(1'b0), .out(_240), .gate(not_11_out));
  Transistor #(.\type ("n")) transistor_103 (.in(1'b0), .out(_240), .gate(not_12_out));
  Transistor #(.\type ("n")) transistor_104 (.in(1'b0), .out(_240), .gate(not_13_out));
  Transistor #(.\type ("n")) transistor_105 (.in(1'b0), .out(_240), .gate(not_14_out));
  Transistor #(.\type ("n")) transistor_106 (.in(1'b0), .out(_240), .gate(V3));
  Transistor #(.\type ("n")) transistor_107 (.in(1'b0), .out(_240), .gate(V2));
  Transistor #(.\type ("n")) transistor_108 (.in(1'b0), .out(_240), .gate(V1));
  Transistor #(.\type ("n")) transistor_109 (.in(1'b0), .out(_240), .gate(V0));
  Pull_Resistor #(.pull(1)) pull_resistor_15 (.node(_255));
  Transistor #(.\type ("n")) transistor_110 (.in(1'b0), .out(_255), .gate(not_2_out));
  Transistor #(.\type ("n")) transistor_111 (.in(1'b0), .out(_255), .gate(not_3_out));
  Transistor #(.\type ("n")) transistor_112 (.in(1'b0), .out(_255), .gate(not_4_out));
  Transistor #(.\type ("n")) transistor_113 (.in(1'b0), .out(_255), .gate(not_5_out));
  Transistor #(.\type ("n")) transistor_114 (.in(1'b0), .out(_255), .gate(not_6_out));
  Transistor #(.\type ("n")) transistor_115 (.in(1'b0), .out(_255), .gate(not_7_out));
  Transistor #(.\type ("n")) transistor_116 (.in(1'b0), .out(_255), .gate(not_8_out));
  Transistor #(.\type ("n")) transistor_117 (.in(1'b0), .out(_255), .gate(not_9_out));
  Pull_Resistor #(.pull(1)) pull_resistor_16 (.node(_261_2));
  Transistor #(.\type ("n")) transistor_118 (.in(1'b0), .out(_261_2), .gate(not_10_out));
  Transistor #(.\type ("n")) transistor_119 (.in(1'b0), .out(_261_2), .gate(V7));
  Transistor #(.\type ("n")) transistor_120 (.in(1'b0), .out(_261_2), .gate(V6));
  Transistor #(.\type ("n")) transistor_121 (.in(1'b0), .out(_261_2), .gate(V5));
  Transistor #(.\type ("n")) transistor_122 (.in(1'b0), .out(_261_2), .gate(V4));
  Transistor #(.\type ("n")) transistor_123 (.in(1'b0), .out(_261_2), .gate(V3));
  Transistor #(.\type ("n")) transistor_124 (.in(1'b0), .out(_261_2), .gate(not_16_out));
  Transistor #(.\type ("n")) transistor_125 (.in(1'b0), .out(_261_2), .gate(V1));
  Transistor #(.\type ("n")) transistor_126 (.in(1'b0), .out(_261_2), .gate(not_18_out));
  Pull_Resistor #(.pull(1)) pull_resistor_17 (.node(_0_63));
  Transistor #(.\type ("n")) transistor_127 (.in(1'b0), .out(_0_63), .gate(H8));
  Transistor #(.\type ("n")) transistor_128 (.in(1'b0), .out(_0_63), .gate(H7));
  Transistor #(.\type ("n")) transistor_129 (.in(1'b0), .out(_0_63), .gate(H6));
  Pull_Resistor #(.pull(1)) pull_resistor_18 (.node(_261_3));
  Transistor #(.\type ("n")) transistor_130 (.in(1'b0), .out(_261_3), .gate(not_10_out));
  Transistor #(.\type ("n")) transistor_131 (.in(1'b0), .out(_261_3), .gate(V7));
  Transistor #(.\type ("n")) transistor_132 (.in(1'b0), .out(_261_3), .gate(V6));
  Transistor #(.\type ("n")) transistor_133 (.in(1'b0), .out(_261_3), .gate(V5));
  Transistor #(.\type ("n")) transistor_134 (.in(1'b0), .out(_261_3), .gate(V4));
  Transistor #(.\type ("n")) transistor_135 (.in(1'b0), .out(_261_3), .gate(V3));
  Transistor #(.\type ("n")) transistor_136 (.in(1'b0), .out(_261_3), .gate(not_16_out));
  Transistor #(.\type ("n")) transistor_137 (.in(1'b0), .out(_261_3), .gate(V1));
  Transistor #(.\type ("n")) transistor_138 (.in(1'b0), .out(_261_3), .gate(not_18_out));
  Pull_Resistor #(.pull(1)) pull_resistor_19 (.node(_256_319));
  Transistor #(.\type ("n")) transistor_139 (.in(1'b0), .out(_256_319), .gate(not_1_out));
  Transistor #(.\type ("n")) transistor_140 (.in(1'b0), .out(_256_319), .gate(H7));
  Transistor #(.\type ("n")) transistor_141 (.in(1'b0), .out(_256_319), .gate(H6));
  Transistor #(.\type ("n")) transistor_142 (.in(1'b0), .out(_256_319), .gate(BLNK));
  Pull_Resistor #(.pull(1)) pull_resistor_20 (.node(_0_255));
  Transistor #(.\type ("n")) transistor_143 (.in(1'b0), .out(_0_255), .gate(H8));
  Transistor #(.\type ("n")) transistor_144 (.in(1'b0), .out(_0_255), .gate(VB));
  Transistor #(.\type ("n")) transistor_145 (.in(1'b0), .out(_0_255), .gate(BLNK));
  Pull_Resistor #(.pull(1)) pull_resistor_21 (.node(_0_1));
  Transistor #(.\type ("n")) transistor_146 (.in(1'b0), .out(_0_1), .gate(H2));
  Transistor #(.\type ("n")) transistor_147 (.in(1'b0), .out(_0_1), .gate(H1));
  Transistor #(.\type ("n")) transistor_148 (.in(1'b0), .out(_0_1), .gate(BLNK));
  Pull_Resistor #(.pull(1)) pull_resistor_22 (.node(_6_7));
  Pull_Resistor #(.pull(1)) pull_resistor_23 (.node(_4_5));
  Transistor #(.\type ("n")) transistor_149 (.in(1'b0), .out(_4_5), .gate(not_7_out));
  Transistor #(.\type ("n")) transistor_150 (.in(1'b0), .out(_6_7), .gate(not_7_out));
  Transistor #(.\type ("n")) transistor_151 (.in(1'b0), .out(_4_5), .gate(H1));
  Transistor #(.\type ("n")) transistor_152 (.in(1'b0), .out(_6_7), .gate(not_8_out));
  Pull_Resistor #(.pull(1)) pull_resistor_24 (.node(_336_340A));
  Transistor #(.\type ("n")) transistor_153 (.in(1'b0), .out(_336_340A), .gate(not_1_out));
  Transistor #(.\type ("n")) transistor_154 (.in(1'b0), .out(_336_340A), .gate(not_3_out));
  Transistor #(.\type ("n")) transistor_155 (.in(1'b0), .out(_336_340A), .gate(H5));
  Transistor #(.\type ("n")) transistor_156 (.in(1'b0), .out(_336_340A), .gate(H4));
  Transistor #(.\type ("n")) transistor_157 (.in(1'b0), .out(_336_340A), .gate(BLNK));
  Pull_Resistor #(.pull(1)) pull_resistor_25 (.node(_336_340B));
  Transistor #(.\type ("n")) transistor_158 (.in(1'b0), .out(_336_340B), .gate(H8));
  Transistor #(.\type ("n")) transistor_159 (.in(1'b0), .out(_336_340B), .gate(BLNK));
  Pull_Resistor #(.pull(1)) pull_resistor_26 (.node(_2_3));
  Transistor #(.\type ("n")) transistor_160 (.in(1'b0), .out(_2_3), .gate(H2));
  Transistor #(.\type ("n")) transistor_161 (.in(1'b0), .out(_2_3), .gate(not_8_out));
  Pull_Resistor #(.pull(1)) pull_resistor_27 (.node(_270));
  Transistor #(.\type ("n")) transistor_162 (.in(1'b0), .out(_270), .gate(not_1_out));
  Transistor #(.\type ("n")) transistor_163 (.in(1'b0), .out(_270), .gate(H7));
  Transistor #(.\type ("n")) transistor_164 (.in(1'b0), .out(_270), .gate(H6));
  Transistor #(.\type ("n")) transistor_165 (.in(1'b0), .out(_270), .gate(H5));
  Transistor #(.\type ("n")) transistor_166 (.in(1'b0), .out(_270), .gate(H4));
  Transistor #(.\type ("n")) transistor_167 (.in(1'b0), .out(_270), .gate(not_6_out));
  Transistor #(.\type ("n")) transistor_168 (.in(1'b0), .out(_270), .gate(not_7_out));
  Transistor #(.\type ("n")) transistor_169 (.in(1'b0), .out(_270), .gate(not_8_out));
  Transistor #(.\type ("n")) transistor_170 (.in(1'b0), .out(_270), .gate(H0));
  Pull_Resistor #(.pull(1)) pull_resistor_28 (.node(_328));
  Transistor #(.\type ("n")) transistor_171 (.in(1'b0), .out(_328), .gate(not_1_out));
  Transistor #(.\type ("n")) transistor_172 (.in(1'b0), .out(_328), .gate(H7));
  Transistor #(.\type ("n")) transistor_173 (.in(1'b0), .out(_328), .gate(not_3_out));
  Transistor #(.\type ("n")) transistor_174 (.in(1'b0), .out(_328), .gate(H5));
  Transistor #(.\type ("n")) transistor_175 (.in(1'b0), .out(_328), .gate(H4));
  Transistor #(.\type ("n")) transistor_176 (.in(1'b0), .out(_328), .gate(not_6_out));
  Transistor #(.\type ("n")) transistor_177 (.in(1'b0), .out(_328), .gate(H2));
  Transistor #(.\type ("n")) transistor_178 (.in(1'b0), .out(_328), .gate(H1));
  Transistor #(.\type ("n")) transistor_179 (.in(1'b0), .out(_328), .gate(H0));
  Pull_Resistor #(.pull(1)) pull_resistor_29 (.node(_279_2));
  Transistor #(.\type ("n")) transistor_180 (.in(1'b0), .out(_279_2), .gate(not_1_out));
  Transistor #(.\type ("n")) transistor_181 (.in(1'b0), .out(_279_2), .gate(H7));
  Transistor #(.\type ("n")) transistor_182 (.in(1'b0), .out(_279_2), .gate(H6));
  Transistor #(.\type ("n")) transistor_183 (.in(1'b0), .out(_279_2), .gate(H5));
  Transistor #(.\type ("n")) transistor_184 (.in(1'b0), .out(_279_2), .gate(not_5_out));
  Transistor #(.\type ("n")) transistor_185 (.in(1'b0), .out(_279_2), .gate(H3));
  Transistor #(.\type ("n")) transistor_186 (.in(1'b0), .out(_279_2), .gate(not_7_out));
  Transistor #(.\type ("n")) transistor_187 (.in(1'b0), .out(_279_2), .gate(not_8_out));
  Transistor #(.\type ("n")) transistor_188 (.in(1'b0), .out(_279_2), .gate(not_9_out));
  Pull_Resistor #(.pull(1)) pull_resistor_30 (.node(_304));
  Pull_Resistor #(.pull(1)) pull_resistor_31 (.node(_323));
  Transistor #(.\type ("n")) transistor_189 (.in(1'b0), .out(_323), .gate(not_1_out));
  Transistor #(.\type ("n")) transistor_190 (.in(1'b0), .out(_304), .gate(not_1_out));
  Transistor #(.\type ("n")) transistor_191 (.in(1'b0), .out(_304), .gate(H7));
  Transistor #(.\type ("n")) transistor_192 (.in(1'b0), .out(_323), .gate(H7));
  Transistor #(.\type ("n")) transistor_193 (.in(1'b0), .out(_304), .gate(H6));
  Transistor #(.\type ("n")) transistor_194 (.in(1'b0), .out(_323), .gate(not_3_out));
  Transistor #(.\type ("n")) transistor_195 (.in(1'b0), .out(_323), .gate(H5));
  Transistor #(.\type ("n")) transistor_196 (.in(1'b0), .out(_304), .gate(not_4_out));
  Transistor #(.\type ("n")) transistor_197 (.in(1'b0), .out(_323), .gate(H4));
  Transistor #(.\type ("n")) transistor_198 (.in(1'b0), .out(_304), .gate(not_5_out));
  Transistor #(.\type ("n")) transistor_199 (.in(1'b0), .out(_304), .gate(H3));
  Transistor #(.\type ("n")) transistor_200 (.in(1'b0), .out(_323), .gate(H3));
  Transistor #(.\type ("n")) transistor_201 (.in(1'b0), .out(_304), .gate(H2));
  Transistor #(.\type ("n")) transistor_202 (.in(1'b0), .out(_323), .gate(H2));
  Transistor #(.\type ("n")) transistor_203 (.in(1'b0), .out(_304), .gate(H1));
  Transistor #(.\type ("n")) transistor_204 (.in(1'b0), .out(_323), .gate(not_8_out));
  Transistor #(.\type ("n")) transistor_205 (.in(1'b0), .out(_304), .gate(H0));
  Transistor #(.\type ("n")) transistor_206 (.in(1'b0), .out(_323), .gate(not_9_out));
  Pull_Resistor #(.pull(1)) pull_resistor_32 (.node(_308));
  Transistor #(.\type ("n")) transistor_207 (.in(1'b0), .out(_308), .gate(not_1_out));
  Transistor #(.\type ("n")) transistor_208 (.in(1'b0), .out(_308), .gate(H7));
  Transistor #(.\type ("n")) transistor_209 (.in(1'b0), .out(_308), .gate(H6));
  Transistor #(.\type ("n")) transistor_210 (.in(1'b0), .out(_308), .gate(not_4_out));
  Transistor #(.\type ("n")) transistor_211 (.in(1'b0), .out(_308), .gate(not_5_out));
  Transistor #(.\type ("n")) transistor_212 (.in(1'b0), .out(_308), .gate(H3));
  Transistor #(.\type ("n")) transistor_213 (.in(1'b0), .out(_308), .gate(not_7_out));
  Transistor #(.\type ("n")) transistor_214 (.in(1'b0), .out(_308), .gate(H1));
  Transistor #(.\type ("n")) transistor_215 (.in(1'b0), .out(_308), .gate(H0));
  Pull_Resistor #(.pull(1)) pull_resistor_33 (.node(_340));
  Transistor #(.\type ("n")) transistor_216 (.in(1'b0), .out(_340), .gate(not_1_out));
  Transistor #(.\type ("n")) transistor_217 (.in(1'b0), .out(_340), .gate(H7));
  Transistor #(.\type ("n")) transistor_218 (.in(1'b0), .out(_340), .gate(not_3_out));
  Transistor #(.\type ("n")) transistor_219 (.in(1'b0), .out(_340), .gate(H5));
  Transistor #(.\type ("n")) transistor_220 (.in(1'b0), .out(_340), .gate(not_5_out));
  Transistor #(.\type ("n")) transistor_221 (.in(1'b0), .out(_340), .gate(H3));
  Transistor #(.\type ("n")) transistor_222 (.in(1'b0), .out(_340), .gate(not_7_out));
  Transistor #(.\type ("n")) transistor_223 (.in(1'b0), .out(_340), .gate(H1));
  Transistor #(.\type ("n")) transistor_224 (.in(1'b0), .out(_340), .gate(H0));
endmodule

module REGISTER_SELECT (
  input  nDBE,
  input  RC,
  input  RS0,
  input  RS1,
  input  RS2,
  input  R_W,
  output nW6_1,
  output nW6_2,
  output nW5_1,
  output nW5_2,
  output nR7,
  output nW7,
  output nW4,
  output nW3,
  output nR2,
  output nW1,
  output nW0,
  output nR4
);

  wire multiplexer_1_out, multiplexer_2_out, nor_1_out, nor_2_out, nor_3_out, nor_4_out, nor_5_out,
       nor_6_out, nor_7_out, nor_8_out, nor_9_out, nor_10_out, nor_11_out, nor_12_out, nor_13_out,
       nor_14_out, nor_15_out, nor_16_out, nor_17_out, not_1_out, not_2_out, not_3_out, not_4_out, not_5_out,
       not_6_out;

  not not_1 (not_1_out, RS0);
  not not_2 (not_2_out, RS1);
  not not_3 (not_3_out, RS2);
  not not_4 (not_4_out, R_W);
  nor nor_1 (nor_1_out, nor_16_out, RC, multiplexer_1_out);
  Multiplexer multiplexer_1 (.in0(not_6_out), .in1(not_5_out), .out(multiplexer_1_out), .sel(nor_15_out));  // open: en
  not not_5 (not_5_out, nor_1_out);
  Multiplexer multiplexer_2 (.in0(not_6_out), .in1(nor_1_out), .out(multiplexer_2_out), .sel(nor_15_out));  // open: en
  nor nor_2 (nor_2_out, multiplexer_2_out, RC, nor_16_out);
  not not_6 (not_6_out, nor_2_out);
  nor nor_3 (nor_3_out, RS0, not_2_out, not_3_out, R_W, nor_1_out);
  nor nor_4 (nor_4_out, RS0, not_2_out, not_3_out, R_W, not_5_out);
  nor nor_5 (nor_5_out, not_1_out, RS1, not_3_out, R_W, nor_1_out);
  nor nor_6 (nor_6_out, not_1_out, RS1, not_3_out, R_W, not_5_out);
  not not_7 (nR7, nor_7_out);
  nor nor_7 (nor_7_out, not_1_out, not_2_out, not_3_out, not_4_out);
  not not_8 (nW7, nor_8_out);
  nor nor_8 (nor_8_out, not_1_out, not_2_out, not_3_out, R_W);
  not not_9 (nW4, nor_9_out);
  nor nor_9 (nor_9_out, RS0, RS1, not_3_out, R_W);
  not not_10 (nW3, nor_10_out);
  nor nor_10 (nor_10_out, not_1_out, not_2_out, RS2, R_W);
  not not_11 (nR2, nor_11_out);
  nor nor_11 (nor_11_out, RS0, not_2_out, RS2, not_4_out);
  nor nor_12 (nor_12_out, not_1_out, RS1, RS2, R_W);
  not not_12 (nW1, nor_12_out);
  not not_13 (nW0, nor_13_out);
  nor nor_13 (nor_13_out, RS0, RS1, RS2, R_W);
  nor nor_14 (nor_14_out, RS0, RS1, not_3_out, not_4_out);
  not not_14 (nR4, nor_14_out);
  nor nor_15 (nor_15_out, nDBE, nor_17_out);
  nor nor_16 (nor_16_out, nDBE, nR2);
  not not_15 (nW6_1, nor_3_out);
  not not_16 (nW6_2, nor_4_out);
  not not_17 (nW5_1, nor_5_out);
  not not_18 (nW5_2, nor_6_out);
  nor nor_17 (nor_17_out, nor_3_out, nor_4_out, nor_5_out, nor_6_out);

  // Notes on the sheet:
  //   1ST
  //   2ND
  //   $2005/$2006 first/second write latch
  //   W5/6
  //   R2
endmodule

module VIDEO_OUT (
  input  CLK,
  input  RES,
  input  nTR,
  input  nTG,
  input  nTB,
  input  PCLK,
  input  CC0,
  input  CC1,
  input  CC2,
  input  CC3,
  input  SYNC,
  input  BURST,
  input  PICTURE,
  input  LL0,
  input  LL1,
  output [10:0] out_16
);

  wire d_latch_1_not_q, d_latch_2_not_q, d_latch_3_not_q, d_latch_4_not_q, d_latch_5_not_q, d_latch_6_not_q,
       d_latch_7_not_q, d_latch_8_q, d_latch_9_q, d_latch_10_not_q, d_latch_11_not_q, d_latch_12_not_q,
       d_latch_13_not_q, d_latch_14_q, d_latch_15_q, d_latch_16_q, d_latch_17_not_q, d_latch_18_q,
       d_latch_19_not_q, d_latch_20_q, d_latch_21_not_q, d_latch_22_q, d_latch_23_not_q, d_latch_24_q,
       d_latch_25_not_q, nor_1_out, nor_2_out, nor_3_out, nor_4_out, nor_5_out, nor_6_out, nor_7_out,
       nor_8_out, nor_9_out, nor_10_out, nor_11_out, nor_12_out, nor_13_out, nor_14_out, nor_15_out,
       nor_16_out, nor_17_out, nor_18_out, nor_19_out, nor_20_out, nor_21_out, nor_22_out, nor_23_out,
       nor_24_out, nor_25_out, nor_26_out, nor_27_out, nor_28_out, nor_29_out, nor_30_out, nor_31_out,
       nor_32_out, nor_33_out, nor_34_out, nor_35_out, nor_36_out, nor_37_out, nor_38_out, nor_39_out,
       nor_40_out, nor_41_out, nor_42_out, nor_43_out, not_1_out, not_2_out, not_3_out, not_4_out, not_5_out,
       not_6_out, not_7_out, not_8_out, not_9_out, not_10_out, not_11_out, not_12_out, not_13_out,
       not_15_out, not_17_out, not_18_out, not_26_out, or_1_out;

  not not_1 (not_1_out, PCLK);
  D_latch d_latch_1 (.EN(PCLK), .D(CC0), .NOT_Q(d_latch_1_not_q));  // open: Q
  D_latch d_latch_2 (.EN(PCLK), .D(CC1), .NOT_Q(d_latch_2_not_q));  // open: Q
  D_latch d_latch_3 (.EN(PCLK), .D(CC2), .NOT_Q(d_latch_3_not_q));  // open: Q
  D_latch d_latch_4 (.EN(PCLK), .D(CC3), .NOT_Q(d_latch_4_not_q));  // open: Q
  nor nor_1 (nor_1_out, nor_7_out, PICTURE);
  not not_2 (not_2_out, LL0);
  not not_3 (not_3_out, LL1);
  nor nor_2 (nor_2_out, d_latch_10_not_q, nTR, nor_24_out);
  nor nor_3 (nor_3_out, d_latch_10_not_q, nTG, nor_34_out);
  nor nor_4 (nor_4_out, d_latch_10_not_q, nTB, nor_11_out);
  D_latch d_latch_5 (.EN(not_1_out), .D(d_latch_1_not_q), .NOT_Q(d_latch_5_not_q));  // open: Q
  D_latch d_latch_6 (.EN(not_1_out), .D(d_latch_2_not_q), .NOT_Q(d_latch_6_not_q));  // open: Q
  D_latch d_latch_7 (.EN(not_1_out), .D(d_latch_3_not_q), .NOT_Q(d_latch_7_not_q));  // open: Q
  D_latch d_latch_8 (.EN(not_1_out), .D(d_latch_4_not_q), .Q(d_latch_8_q));  // open: NOT_Q
  D_latch d_latch_9 (.EN(not_1_out), .D(or_1_out), .Q(d_latch_9_q));  // open: NOT_Q
  or or_1 (or_1_out, SYNC, BURST, nor_1_out);
  not not_4 (not_4_out, SYNC);
  nor nor_5 (nor_5_out, nor_2_out, nor_3_out, nor_4_out);
  not not_5 (not_5_out, nor_5_out);
  nor nor_6 (nor_6_out, d_latch_8_q, d_latch_9_q);
  D_latch d_latch_10 (.EN(not_1_out), .D(nor_1_out), .NOT_Q(d_latch_10_not_q));  // open: Q
  D_latch d_latch_11 (.EN(not_1_out), .D(not_4_out), .NOT_Q(d_latch_11_not_q));  // open: Q
  D_latch d_latch_12 (.EN(not_1_out), .D(BURST), .NOT_Q(d_latch_12_not_q));  // open: Q
  nor nor_7 (nor_7_out, d_latch_6_not_q, d_latch_7_not_q, nor_6_out);
  not not_6 (not_6_out, d_latch_19_not_q);
  not not_7 (not_7_out, d_latch_5_not_q);
  not not_8 (not_8_out, d_latch_6_not_q);
  not not_9 (not_9_out, d_latch_7_not_q);
  not not_10 (not_10_out, nor_6_out);
  D_latch d_latch_13 (.EN(not_1_out), .D(or_1_out), .NOT_Q(d_latch_13_not_q));  // open: Q
  not not_11 (not_11_out, nor_8_out);
  nor nor_8 (nor_8_out, d_latch_10_not_q, not_2_out, not_3_out);
  not not_12 (not_12_out, CLK);
  not not_13 (not_13_out, nor_9_out);
  nor nor_9 (nor_9_out, d_latch_10_not_q, LL0, LL1);
  D_latch d_latch_14 (.EN(not_12_out), .D(not_6_out), .Q(d_latch_14_q));  // open: NOT_Q
  nor nor_10 (nor_10_out, not_6_out, nor_21_out);
  not not_14 (out_16[0], not_5_out);
  not not_15 (not_15_out, d_latch_13_not_q);
  not not_16 (out_16[10], d_latch_11_not_q);
  nor nor_11 (nor_11_out, d_latch_14_q, RES);
  nor nor_12 (nor_12_out, nor_11_out, not_7_out, not_8_out, d_latch_7_not_q, nor_6_out);
  not not_17 (not_17_out, nor_13_out);
  nor nor_13 (nor_13_out, d_latch_10_not_q, not_2_out, LL1);
  D_latch d_latch_15 (.EN(CLK), .D(nor_11_out), .Q(d_latch_15_q));  // open: NOT_Q
  not not_18 (not_18_out, nor_14_out);
  nor nor_14 (nor_14_out, d_latch_10_not_q, LL0, not_3_out);
  nor nor_15 (nor_15_out, d_latch_15_q, nor_10_out);
  nor nor_16 (nor_16_out, nor_15_out, d_latch_5_not_q, not_8_out, d_latch_7_not_q, not_10_out);
  D_latch d_latch_16 (.EN(not_12_out), .D(nor_15_out), .Q(d_latch_16_q));  // open: NOT_Q
  nor nor_17 (nor_17_out, nor_43_out, d_latch_12_not_q);
  nor nor_18 (nor_18_out, d_latch_12_not_q, nor_17_out);
  nor nor_19 (nor_19_out, d_latch_16_q, RES);
  nor nor_20 (nor_20_out, nor_19_out, not_7_out, d_latch_6_not_q, not_9_out, nor_6_out);
  not not_19 (out_16[6], nor_17_out);
  not not_20 (out_16[9], nor_18_out);
  D_latch d_latch_17 (.EN(CLK), .D(nor_19_out), .NOT_Q(d_latch_17_not_q));  // open: Q
  nor nor_21 (nor_21_out, d_latch_17_not_q, d_latch_5_not_q, d_latch_6_not_q, not_9_out, not_10_out);
  or or_2 (out_16[7], not_15_out, not_26_out);
  D_latch d_latch_18 (.EN(not_12_out), .D(d_latch_17_not_q), .Q(d_latch_18_q));  // open: NOT_Q
  nor nor_22 (nor_22_out, nor_43_out, not_11_out);
  nor nor_23 (nor_23_out, not_11_out, nor_22_out);
  nor nor_24 (nor_24_out, d_latch_18_q, RES);
  nor nor_25 (nor_25_out, nor_24_out, not_7_out, not_8_out, not_9_out, nor_6_out);
  not not_21 (out_16[4], nor_22_out);
  not not_22 (out_16[8], nor_23_out);
  D_latch d_latch_19 (.EN(CLK), .D(nor_24_out), .NOT_Q(d_latch_19_not_q));  // open: Q
  D_latch d_latch_20 (.EN(not_12_out), .D(d_latch_19_not_q), .Q(d_latch_20_q));  // open: NOT_Q
  nor nor_26 (nor_26_out, d_latch_19_not_q, d_latch_5_not_q, not_8_out, not_9_out, not_10_out);
  nor nor_27 (nor_27_out, nor_43_out, not_13_out);
  nor nor_28 (nor_28_out, not_13_out, nor_27_out);
  nor nor_29 (nor_29_out, d_latch_20_q, RES);
  not not_23 (out_16[1], nor_27_out);
  not not_24 (out_16[2], nor_28_out);
  D_latch d_latch_21 (.EN(CLK), .D(nor_29_out), .NOT_Q(d_latch_21_not_q));  // open: Q
  nor nor_30 (nor_30_out, nor_29_out, not_7_out, d_latch_6_not_q, d_latch_7_not_q, not_10_out);
  D_latch d_latch_22 (.EN(not_12_out), .D(d_latch_21_not_q), .Q(d_latch_22_q));  // open: NOT_Q
  nor nor_31 (nor_31_out, d_latch_21_not_q, d_latch_5_not_q, d_latch_6_not_q, not_9_out, nor_6_out);
  nor nor_32 (nor_32_out, nor_43_out, not_18_out);
  nor nor_33 (nor_33_out, not_18_out, nor_32_out);
  D_latch d_latch_23 (.EN(CLK), .D(nor_34_out), .NOT_Q(d_latch_23_not_q));  // open: Q
  nor nor_34 (nor_34_out, d_latch_22_q, RES);
  not not_25 (out_16[3], nor_32_out);
  not not_26 (not_26_out, nor_33_out);
  D_latch d_latch_24 (.EN(not_12_out), .D(d_latch_23_not_q), .Q(d_latch_24_q));  // open: NOT_Q
  nor nor_35 (nor_35_out, nor_34_out, not_7_out, not_8_out, d_latch_7_not_q, not_10_out);
  nor nor_36 (nor_36_out, d_latch_24_q, RES);
  not not_27 (out_16[1], nor_37_out);
  nor nor_37 (nor_37_out, nor_43_out, not_17_out);
  nor nor_38 (nor_38_out, not_17_out, nor_37_out);
  not not_28 (out_16[5], nor_38_out);
  D_latch d_latch_25 (.EN(CLK), .D(nor_36_out), .NOT_Q(d_latch_25_not_q));  // open: Q
  nor nor_39 (nor_39_out, d_latch_23_not_q, d_latch_5_not_q, not_8_out, not_9_out, nor_6_out);
  nor nor_40 (nor_40_out, nor_36_out, not_7_out, d_latch_6_not_q, not_9_out, not_10_out);
  nor nor_41 (nor_41_out, d_latch_25_not_q, d_latch_5_not_q, d_latch_6_not_q, d_latch_7_not_q, not_10_out);
  nor nor_42 (nor_42_out, not_7_out, not_8_out, not_9_out, not_10_out);
  nor nor_43 (nor_43_out, nor_41_out, nor_40_out, nor_39_out, nor_35_out, nor_31_out, nor_30_out, nor_42_out, nor_26_out, nor_25_out, nor_21_out, nor_20_out, nor_16_out, nor_12_out);

  // Notes on the sheet:
  //   Emphasis
  //   TINT
  //   /POUT
  //   /POUT
  //   0
  //   1
  //   2
  //   3
  //   /PB
  //   /PR
  //   /PG
  //   /LU3
  //   P123
  //   TINT
  //   Color 1D (black)
  //   Synch
  //   Color burst
  //   /LU0
  //   /LU1
  //   /LU2
  //   /PZ
  //   /PZ
endmodule

module CPU_DATA_PAD (
  input  WR,
  input  RD,
  input  DB_out,
  input  DATA_PPU,
  output PPU_DATA,
  output DB_in
);

  assign PPU_DATA = RD ? DB_out : 1'bz;  // Controlled_Buffer controlled_buffer_1
  assign DB_in = WR ? DATA_PPU : 1'bz;  // Controlled_Buffer controlled_buffer_2
endmodule
